// Logisim project RANDOM.circ as structural Verilog: 2 circuits, main circuit main
module main (
  input  BRK6E,
  input  _0_ADL0,
  input  D0,
  input  D1,
  input  D2,
  input  D3,
  input  D4,
  input  D5,
  input  D6,
  input  D7,
  input  D8,
  input  D9,
  input  D10,
  input  D11,
  input  D12,
  input  D13,
  input  D14,
  input  D15,
  input  D16,
  input  D17,
  input  D18,
  input  D19,
  input  D20,
  input  D21,
  input  D22,
  input  D23,
  input  D24,
  input  D25,
  input  D26,
  input  D27,
  input  D28,
  input  D29,
  input  D30,
  input  D31,
  input  D32,
  input  D33,
  input  D34,
  input  D35,
  input  D36,
  input  D37,
  input  D38,
  input  D39,
  input  D40,
  input  D41,
  input  D42,
  input  D43,
  input  D44,
  input  D45,
  input  D46,
  input  D47,
  input  D48,
  input  D49,
  input  D50,
  input  D51,
  input  D52,
  input  D53,
  input  D54,
  input  D55,
  input  D56,
  input  D57,
  input  D58,
  input  D59,
  input  D60,
  input  D61,
  input  D62,
  input  D63,
  input  D64,
  input  D65,
  input  D66,
  input  D67,
  input  D68,
  input  D69,
  input  D70,
  input  D71,
  input  D72,
  input  D73,
  input  D74,
  input  D75,
  input  D76,
  input  D77,
  input  D78,
  input  D79,
  input  D80,
  input  D81,
  input  D82,
  input  D83,
  input  D84,
  input  D85,
  input  D86,
  input  D87,
  input  D88,
  input  D89,
  input  D90,
  input  D91,
  input  D92,
  input  D93,
  input  D94,
  input  D95,
  input  D96,
  input  D97,
  input  D98,
  input  D99,
  input  D100,
  input  D101,
  input  D102,
  input  D103,
  input  D104,
  input  D105,
  input  D106,
  input  D107,
  input  D108,
  input  D109,
  input  D110,
  input  D111,
  input  D112,
  input  D113,
  input  D114,
  input  D115,
  input  D116,
  input  D117,
  input  D118,
  input  D119,
  input  D120,
  input  D121,
  input  D122,
  input  D123,
  input  D124,
  input  D125,
  input  D126,
  input  D127,
  input  D128,
  input  D129,
  input  SO,
  input  RESP,
  input  DORES,
  input  ACR,
  input  RDY,
  input  B_OUT,
  input  nIMPLIED,
  input  nTWOCYCLE,
  input  nC_OUT,
  input  nV_OUT,
  input  nN_OUT,
  input  nZ_OUT,
  input  nD_OUT,
  input  nIR5,
  input  DB7,
  output BRK5,
  output BR2,
  output nready,
  output ADH_ABH,
  output ADL_ABL,
  output Y_SB,
  output X_SB,
  output SB_Y,
  output SB_X,
  output S_SB,
  output S_ADL,
  output SB_S,
  output S_S,
  output NDB_ADD,
  output DB_ADD,
  output _0_ADD,
  output SB_ADD,
  output ADL_ADD,
  output ANDS,
  output EORS,
  output ORS,
  output nACIN,
  output SRS,
  output SUMS,
  output nDAA,
  output ADD_SB7,
  output ADD_SB06,
  output ADD_ADL,
  output nDSA,
  output _0_ADH0,
  output SB_DB,
  output SB_AC,
  output SB_ADH,
  output _0_ADH17,
  output AC_SB,
  output AC_DB,
  output ADH_PCH,
  output PCH_PCH,
  output PCH_DB,
  output PCL_DB,
  output PCH_ADH,
  output PCL_PCL,
  output PCL_ADL,
  output ADL_PCL,
  output DL_ADL,
  output DL_ADH,
  output DL_DB,
  output P_DB,
  output ACR_C,
  output AVR_V,
  output DBZ_Z,
  output DB_N,
  output DB_P,
  output DB_C,
  output DB_V,
  output IR5_C,
  output IR5_I,
  output IR5_D,
  output _0_V,
  output _1_V,
  output RW,
  output SYNC,
  output _1_PC,
  output FETCH,
  output _0_IR,
  output nT0X,
  output nT1X,
  output nT2,
  output nT3,
  output nT4,
  output nT5,
  output RD
);

  wire and_1_out, and_2_out, and_3_out, and_4_out, and_5_out, and_6_out, and_7_out, and_8_out, and_9_out,
       and_10_out, and_11_out, and_12_out, and_14_out, and_15_out, and_16_out, and_17_out, and_18_out,
       and_19_out, and_20_out, and_21_out, and_22_out, and_23_out, and_24_out, and_25_out, and_26_out,
       and_27_out, and_30_out, and_31_out, and_32_out, and_33_out, buffer_5_out, buffer_6_out, buffer_7_out,
       buffer_8_out, buffer_11_out, buffer_12_out, buffer_13_out, buffer_14_out, buffer_15_out,
       buffer_16_out, buffer_17_out, buffer_28_out, buffer_31_out, buffer_32_out, buffer_33_out,
       buffer_34_out, buffer_38_out, buffer_40_out, d_latch_1_out, d_latch_2_out_2, d_latch_3_out,
       d_latch_4_out, d_latch_5_out, d_latch_6_out, d_latch_7_out_2, d_latch_8_out, d_latch_9_out_2,
       d_latch_10_out, d_latch_11_out, d_latch_12_out_2, d_latch_13_out_2, d_latch_14_out, d_latch_15_out,
       d_latch_16_out_2, d_latch_17_out, d_latch_18_out_2, d_latch_19_out, d_latch_20_out, d_latch_21_out,
       d_latch_22_out, d_latch_23_out, d_latch_24_out, d_latch_25_out, d_latch_26_out, d_latch_27_out,
       d_latch_28_out, d_latch_29_out_2, d_latch_30_out, d_latch_31_out_2, d_latch_32_out, d_latch_33_out_2,
       d_latch_34_out, d_latch_35_out_2, d_latch_36_out, d_latch_37_out_2, d_latch_38_out_2,
       d_latch_39_out_2, d_latch_40_out_2, d_latch_41_out, d_latch_42_out, d_latch_43_out, d_latch_44_out_2,
       d_latch_45_out, d_latch_46_out_2, d_latch_47_out_2, d_latch_48_out_2, d_latch_49_out_2,
       d_latch_50_out, d_latch_51_out_2, d_latch_52_out, d_latch_53_out_2, d_latch_54_out_2,
       d_latch_55_out_2, d_latch_56_out_2, d_latch_57_out_2, d_latch_58_out_2, d_latch_59_out,
       d_latch_60_out, d_latch_61_out, d_latch_62_out, d_latch_63_out_2, d_latch_64_out_2, d_latch_65_out_2,
       d_latch_66_out_2, d_latch_67_out_2, d_latch_68_out_2, d_latch_69_out_2, d_latch_70_out_2,
       d_latch_71_out_2, d_latch_72_out_2, d_latch_73_out_2, d_latch_74_out_2, d_latch_75_out_2,
       d_latch_76_out_2, d_latch_77_out_2, d_latch_78_out_2, d_latch_79_out_2, d_latch_80_out_2,
       d_latch_81_out_2, d_latch_82_out_2, d_latch_83_out_2, d_latch_84_out_2, d_latch_85_out_2,
       d_latch_86_out_2, d_latch_87_out_2, d_latch_90_out_2, d_latch_91_out_2, d_latch_92_out_2,
       d_latch_93_out_2, d_latch_94_out_2, d_latch_95_out_2, d_latch_96_out_2, d_latch_97_out_2,
       d_latch_98_out_2, d_latch_99_out_2, d_latch_100_out_2, d_latch_101_out_2, d_latch_102_out_2,
       d_latch_103_out_2, d_latch_104_out_2, d_latch_105_out_2, d_latch_106_out_2, d_latch_110_out,
       d_latch_117_out, d_latch_118_out, d_latch_119_out, d_latch_120_out, d_latch_121_out, d_latch_122_out,
       d_latch_123_out, d_latch_124_out, d_latch_125_out, d_latch_126_out, nand_1_out, nand_2_out,
       nand_3_out, nand_4_out, nand_5_out, nand_6_out, nand_7_out, nand_8_out, nand_9_out, nand_10_out,
       nand_11_out, nand_12_out, nand_13_out, nand_14_out, nand_15_out, nand_16_out, nand_17_out,
       nand_18_out, nand_19_out, nand_20_out, nand_21_out, nand_22_out, nand_23_out, nand_24_out,
       nand_25_out, nand_26_out, nand_27_out, nand_28_out, nand_29_out, nand_30_out, nand_31_out,
       nand_32_out, nand_33_out, nand_34_out, nand_35_out, nand_37_out, nand_38_out, nand_39_out,
       nand_40_out, nand_41_out, nand_42_out, nand_43_out, nor_1_out, nor_2_out, nor_3_out, nor_4_out,
       nor_5_out, nor_6_out, nor_7_out, nor_8_out, nor_9_out, nor_10_out, nor_11_out, nor_12_out, nor_13_out,
       nor_14_out, nor_15_out, nor_16_out, nor_17_out, nor_18_out, nor_19_out, nor_20_out, nor_21_out,
       nor_22_out, nor_23_out, nor_24_out, nor_25_out, nor_26_out, nor_27_out, nor_28_out, nor_29_out,
       nor_30_out, nor_31_out, nor_32_out, nor_33_out, nor_34_out, nor_35_out, nor_36_out, nor_37_out,
       nor_38_out, nor_39_out, nor_40_out, nor_41_out, nor_42_out, nor_43_out, nor_44_out, nor_45_out,
       nor_46_out, nor_47_out, nor_48_out, nor_49_out, nor_50_out, nor_51_out, nor_52_out, nor_53_out,
       nor_54_out, nor_55_out, nor_56_out, nor_57_out, nor_58_out, nor_59_out, nor_60_out, nor_61_out,
       nor_62_out, nor_63_out, nor_64_out, nor_65_out, nor_66_out, nor_67_out, nor_68_out, nor_69_out,
       nor_70_out, nor_71_out, nor_72_out, nor_73_out, nor_74_out, nor_75_out, nor_76_out, nor_77_out,
       nor_78_out, nor_79_out, nor_80_out, nor_81_out, nor_82_out, nor_84_out, nor_85_out, nor_86_out,
       nor_87_out, nor_88_out, nor_89_out, nor_90_out, nor_91_out, nor_92_out, nor_93_out, nor_94_out,
       nor_95_out, nor_96_out, nor_97_out, nor_98_out, nor_99_out, nor_100_out, nor_101_out, nor_102_out,
       nor_103_out, nor_104_out, nor_105_out, nor_106_out, nor_107_out, nor_108_out, nor_109_out, not_1_out,
       not_2_out, not_3_out, not_4_out, not_5_out, not_6_out, not_7_out, not_8_out, not_9_out, not_10_out,
       not_11_out, not_12_out, not_13_out, not_14_out, not_15_out, not_16_out, not_17_out, not_18_out,
       not_19_out, not_20_out, not_21_out, not_22_out, not_23_out, not_24_out, not_25_out, not_26_out,
       not_27_out, not_28_out, not_29_out, not_30_out, not_31_out, not_32_out, not_33_out, not_34_out,
       not_35_out, not_36_out, not_37_out, not_38_out, not_39_out, not_40_out, not_41_out, not_42_out,
       not_43_out, not_44_out, not_45_out, not_46_out, not_47_out, not_48_out, not_49_out, not_50_out,
       not_51_out, not_52_out, not_53_out, not_54_out, not_55_out, not_56_out, not_57_out, not_58_out,
       not_59_out, not_60_out, not_61_out, not_62_out, not_63_out, not_64_out, not_65_out, not_66_out,
       not_67_out, not_68_out, not_69_out, not_70_out, not_71_out, not_72_out, not_73_out, not_74_out,
       not_75_out, not_76_out, not_77_out, not_78_out, not_79_out, not_80_out, not_81_out, not_82_out,
       not_83_out, not_84_out, not_85_out, not_86_out, not_87_out, not_88_out, not_89_out, not_90_out,
       not_91_out, not_93_out, not_94_out, not_95_out, not_96_out, not_98_out, not_99_out, not_100_out,
       not_101_out, not_102_out, not_103_out, not_104_out, not_105_out, not_106_out, not_107_out,
       not_108_out, not_109_out, not_110_out, not_111_out, not_112_out, not_113_out, not_114_out,
       not_115_out, not_116_out, not_117_out, not_119_out, not_120_out, not_121_out, not_122_out,
       not_123_out, not_124_out, not_125_out, not_126_out, not_127_out, not_128_out, not_129_out,
       not_130_out, not_131_out, not_132_out, not_133_out, not_134_out, not_135_out, not_136_out,
       not_137_out, not_138_out, not_139_out, not_140_out, not_141_out, not_142_out, not_143_out,
       not_144_out, not_145_out, not_146_out, not_147_out, not_148_out, not_149_out, or_1_out, or_2_out,
       or_3_out, or_4_out, or_5_out, or_6_out, or_7_out, or_8_out, or_9_out, or_10_out, PHI0_out, xnor_1_out;

  Clock PHI0 (.out(PHI0_out));
  not not_1 (not_1_out, d_latch_18_out_2);
  nor nor_1 (nor_1_out, D14, D15, D16);
  not not_2 (not_2_out, D17);
  nor nor_2 (nor_2_out, D18, D19, D20);
  nor nor_3 (nor_3_out, D52, D53);
  nor nor_4 (nor_4_out, D129, D90);
  nor nor_5 (nor_5_out, D100, D101, D102, D103, D104, D105);
  not not_3 (not_3_out, ACR);
  nor nor_6 (nor_6_out, not_1_out, d_latch_2_out_2);
  nor nor_7 (nor_7_out, D1, D2, D3, D4, D5);
  nor nor_8 (nor_8_out, D8, D9, D10, D11, D13);
  not not_4 (not_4_out, D29);
  not not_5 (not_5_out, D93);
  nor nor_9 (nor_9_out, D71, D72);
  not not_6 (not_6_out, D97);
  nor nor_10 (nor_10_out, D111, D122, D123, D124, D125);
  not not_7 (not_7_out, D129);
  not not_8 (not_8_out, DB7);
  D_LATCH d_latch_1 (.EN(PHI0_out), .in(D80), .out(d_latch_1_out));  // open: out_2
  not not_9 (not_9_out, d_latch_1_out);
  nand nand_1 (nand_1_out, not_3_out, not_1_out);
  not not_10 (not_10_out, nor_6_out);
  D_LATCH d_latch_2 (.EN(PHI0_out), .in(d_latch_7_out_2), .out_2(d_latch_2_out_2));  // open: out
  not not_11 (not_11_out, D7);
  nand nand_2 (nand_2_out, nor_1_out, nor_2_out);
  nor nor_11 (nor_11_out, D21, D22, D23, D24, D25, D26);
  not not_12 (not_12_out, not_4_out);
  nor nor_12 (nor_12_out, nready, D32);
  not not_13 (not_13_out, nor_12_out);
  not not_14 (not_14_out, D34);
  nor nor_13 (nor_13_out, not_5_out, not_34_out);
  not not_15 (not_15_out, nor_14_out);
  nor nor_14 (nor_14_out, D69, D70);
  not not_16 (not_16_out, D75);
  nand nand_3 (nand_3_out, D76, d_latch_51_out_2);
  and and_1 (and_1_out, D128, not_7_out);
  D_LATCH d_latch_3 (.EN(not_17_out), .in(nor_71_out), .out(d_latch_3_out));  // open: out_2
  not not_17 (not_17_out, PHI0_out);
  not not_18 (not_18_out, PHI0_out);
  D_LATCH d_latch_4 (.EN(not_18_out), .in(nTWOCYCLE), .out(d_latch_4_out));  // open: out_2
  not not_19 (not_19_out, PHI0_out);
  D_LATCH d_latch_5 (.EN(not_19_out), .in(not_149_out), .out(d_latch_5_out));  // open: out_2
  nand nand_4 (nand_4_out, not_8_out, d_latch_1_out);
  and and_2 (and_2_out, nand_4_out, nand_5_out);
  nand nand_5 (nand_5_out, not_9_out, d_latch_6_out);
  not not_20 (not_20_out, PHI0_out);
  and and_3 (and_3_out, nand_1_out, not_10_out);
  nand nand_6 (nand_6_out, nor_27_out, D0);
  nand nand_7 (nand_7_out, D6, D7);
  nand nand_8 (nand_8_out, D6, not_11_out);
  nand nand_9 (nand_9_out, nor_27_out, D12);
  not not_21 (not_21_out, PHI0_out);
  nand nand_10 (nand_10_out, D33, not_14_out);
  nor nor_15 (nor_15_out, D35, D36, D37, D38, D39, nready);
  nor nor_16 (nor_16_out, D39, D40, D41, D42, D43);
  nand nand_11 (nand_11_out, D44, d_latch_51_out_2);
  not not_22 (not_22_out, nor_17_out);
  nor nor_17 (nor_17_out, D49, D50, nor_13_out);
  nor nor_18 (nor_18_out, not_56_out, d_latch_51_out_2);
  not not_23 (not_23_out, nor_20_out);
  nor nor_19 (nor_19_out, D58, D59, D60, D61, D62, D63, D64);
  not not_24 (not_24_out, D64);
  not not_25 (not_25_out, RDY);
  not not_26 (not_26_out, and_4_out);
  and and_4 (and_4_out, not_16_out, nand_3_out);
  nor nor_20 (nor_20_out, D81, D82);
  nor nor_21 (nor_21_out, D83, D129);
  nor nor_22 (nor_22_out, D85, D86, D84, D26, D87, D88, D89);
  nor nor_23 (nor_23_out, D89, nor_4_out, D91, D84);
  not not_27 (not_27_out, nor_23_out);
  nor nor_24 (nor_24_out, D94, D95, D96);
  nor nor_25 (nor_25_out, D91, D92);
  nor nor_26 (nor_26_out, D98, D99);
  nor nor_27 (nor_27_out, not_6_out, nor_10_out);
  nor nor_28 (nor_28_out, D106, D107);
  not not_28 (not_28_out, D113);
  nor nor_29 (nor_29_out, D114, D115);
  and and_5 (and_5_out, d_latch_3_out, d_latch_4_out);
  not not_29 (not_29_out, PHI0_out);
  D_LATCH d_latch_6 (.EN(PHI0_out), .in(d_latch_12_out_2), .out(d_latch_6_out));  // open: out_2
  D_LATCH d_latch_7 (.EN(not_20_out), .in(and_3_out), .out_2(d_latch_7_out_2));  // open: out
  D_LATCH d_latch_8 (.EN(not_21_out), .in(nready), .out(d_latch_8_out));  // open: out_2
  and and_6 (and_6_out, nand_10_out, nor_15_out);
  and and_7 (and_7_out, nor_16_out, nand_11_out);
  nor nor_30 (nor_30_out, nor_18_out, nC_OUT);
  nor nor_31 (nor_31_out, D57, not_23_out);
  nand nand_12 (nand_12_out, D65, not_24_out);
  nor nor_32 (nor_32_out, D66, D67, D68, not_15_out);
  D_LATCH d_latch_9 (.EN(PHI0_out), .in(not_25_out), .out_2(d_latch_9_out_2));  // open: out
  not not_30 (not_30_out, PHI0_out);
  D_LATCH d_latch_10 (.EN(PHI0_out), .in(not_28_out), .out(d_latch_10_out));  // open: out_2
  D_LATCH d_latch_11 (.EN(PHI0_out), .in(nor_29_out), .out(d_latch_11_out));  // open: out_2
  nor nor_33 (nor_33_out, RDY, d_latch_15_out);
  nor nor_34 (nor_34_out, d_latch_14_out, and_9_out, d_latch_28_out);
  nand nand_13 (nand_13_out, not_6_out, nor_28_out);
  or or_1 (or_1_out, and_5_out, d_latch_5_out);
  D_LATCH d_latch_12 (.EN(not_29_out), .in(and_2_out), .out_2(d_latch_12_out_2));  // open: out
  not not_31 (not_31_out, and_7_out);
  not not_32 (not_32_out, nor_30_out);
  and and_8 (and_8_out, nand_12_out, nor_32_out);
  D_LATCH d_latch_13 (.EN(not_30_out), .in(d_latch_9_out_2), .out_2(d_latch_13_out_2));  // open: out
  D_LATCH d_latch_14 (.EN(PHI0_out), .in(nor_33_out), .out(d_latch_14_out));  // open: out_2
  not not_33 (not_33_out, PHI0_out);
  D_LATCH d_latch_15 (.EN(not_33_out), .in(nor_34_out), .out(d_latch_15_out));  // open: out_2
  and and_9 (and_9_out, nand_13_out, DORES);
  nor nor_35 (nor_35_out, d_latch_19_out, d_latch_20_out);
  not not_34 (not_34_out, d_latch_12_out_2);
  not not_35 (not_35_out, PHI0_out);
  D_LATCH d_latch_16 (.EN(not_35_out), .in(nready), .out_2(d_latch_16_out_2));  // open: out
  and and_10 (and_10_out, nand_6_out, nor_7_out, nand_7_out);
  and and_11 (and_11_out, nand_8_out, nor_8_out, nand_9_out);
  nand nand_14 (nand_14_out, D0, nor_27_out);
  nand nand_15 (nand_15_out, nor_27_out, D12);
  nand nand_16 (nand_16_out, D21, not_36_out);
  not not_36 (not_36_out, d_latch_8_out);
  not not_37 (not_37_out, D48);
  nor nor_36 (nor_36_out, not_31_out, BRK6E, D48, D45, D46, D47);
  or or_2 (or_2_out, not_32_out, nor_3_out);
  nand nand_17 (nand_17_out, or_2_out, not_38_out);
  not not_38 (not_38_out, D54);
  nor nor_37 (nor_37_out, D112, D116, D117, D118, D119);
  and and_12 (and_12_out, nor_37_out, nand_18_out);
  nand nand_18 (nand_18_out, D107, not_96_out);
  buf buffer_1 (nready, d_latch_14_out);
  and and_13 (nT0X, or_1_out, not_39_out);
  not not_39 (not_39_out, nor_35_out);
  nor nor_38 (nor_38_out, d_latch_19_out, nready);
  not not_40 (not_40_out, D121);
  not not_41 (not_41_out, D126);
  not not_42 (not_42_out, D126);
  not not_43 (not_43_out, D121);
  nor nor_39 (nor_39_out, D80, D93);
  and and_14 (and_14_out, nand_14_out, nand_15_out);
  and and_15 (and_15_out, nand_16_out, not_44_out);
  not not_44 (not_44_out, D35);
  nor nor_40 (nor_40_out, nor_11_out, d_latch_8_out);
  nor nor_41 (nor_41_out, not_37_out, nready);
  nor nor_42 (nor_42_out, D30, D31, D47, nready, nor_40_out, not_31_out, D45, BRK6E, D48);
  not not_45 (not_45_out, D47);
  not not_46 (not_46_out, nor_36_out);
  not not_47 (not_47_out, nor_19_out);
  nor nor_43 (nor_43_out, d_latch_13_out_2, D73);
  not not_48 (not_48_out, nor_9_out);
  nor nor_44 (nor_44_out, D77, D78);
  nor nor_45 (nor_45_out, nor_24_out, d_latch_8_out);
  not not_49 (not_49_out, not_56_out);
  D_LATCH d_latch_17 (.EN(PHI0_out), .in(D109), .out(d_latch_17_out));  // open: out_2
  not not_50 (not_50_out, PHI0_out);
  nor nor_46 (nor_46_out, nC_OUT, D126, not_40_out);
  nor nor_47 (nor_47_out, nV_OUT, D121, not_41_out);
  nor nor_48 (nor_48_out, nN_OUT, not_42_out, not_43_out);
  nor nor_49 (nor_49_out, nZ_OUT, D121, D126);
  not not_51 (not_51_out, nor_39_out);
  D_LATCH d_latch_18 (.EN(PHI0_out), .in(d_latch_16_out_2), .out_2(d_latch_18_out_2));  // open: out
  not not_52 (not_52_out, d_latch_8_out);
  nor nor_50 (nor_50_out, nor_40_out, nor_41_out, D13);
  nor nor_51 (nor_51_out, not_45_out, and_6_out);
  nor nor_52 (nor_52_out, not_47_out, nand_2_out, not_96_out, not_15_out);
  nand nand_19 (nand_19_out, nor_9_out, not_53_out);
  not not_53 (not_53_out, nor_43_out);
  nor nor_53 (nor_53_out, not_48_out, nready);
  nor nor_54 (nor_54_out, d_latch_51_out_2, not_96_out);
  not not_54 (not_54_out, D74);
  nand nand_20 (nand_20_out, D79, nor_27_out);
  nor nor_55 (nor_55_out, nor_45_out, not_49_out);
  nor nor_56 (nor_56_out, not_49_out, nor_24_out);
  not not_55 (not_55_out, d_latch_8_out);
  nor nor_57 (nor_57_out, nready, nor_109_out);
  D_LATCH d_latch_19 (.EN(PHI0_out), .in(nT0X), .out(d_latch_19_out));  // open: out_2
  not not_56 (not_56_out, nT0X);
  D_LATCH d_latch_20 (.EN(not_50_out), .in(nor_38_out), .out(d_latch_20_out), .out_2(nT1X));
  nor nor_58 (nor_58_out, nor_46_out, nor_47_out, nor_48_out, nor_49_out);
  nand nand_21 (nand_21_out, D80, and_19_out);
  nor nor_59 (nor_59_out, and_18_out, not_51_out);
  not not_57 (not_57_out, nor_59_out);
  nor nor_60 (nor_60_out, D93, d_latch_18_out_2);
  nand nand_22 (nand_22_out, not_52_out, and_3_out);
  not not_58 (not_58_out, not_26_out);
  nand nand_23 (nand_23_out, nor_53_out, nor_54_out);
  and and_16 (and_16_out, not_54_out, nand_20_out);
  D_LATCH d_latch_21 (.EN(PHI0_out), .in(nor_44_out), .out(d_latch_21_out));  // open: out_2
  not not_59 (not_59_out, nor_67_out);
  nor nor_61 (nor_61_out, not_59_out, not_56_out, D84);
  nand nand_24 (nand_24_out, D93, not_55_out);
  D_LATCH d_latch_22 (.EN(PHI0_out), .in(nor_25_out), .out(d_latch_22_out));  // open: out_2
  nor nor_62 (nor_62_out, RESP, nor_99_out, nor_57_out);
  nand nand_25 (nand_25_out, nIR5, nor_58_out);
  nor nor_63 (nor_63_out, nIR5, nor_58_out);
  and and_17 (and_17_out, nand_21_out, not_57_out);
  D_LATCH d_latch_23 (.EN(PHI0_out), .in(nor_60_out), .out(d_latch_23_out));  // open: out_2
  nor nor_64 (nor_64_out, nand_22_out, nor_87_out);
  D_LATCH d_latch_24 (.EN(PHI0_out), .in(nor_51_out), .out(d_latch_24_out));  // open: out_2
  D_LATCH d_latch_25 (.EN(PHI0_out), .in(not_31_out), .out(d_latch_25_out));  // open: out_2
  D_LATCH d_latch_26 (.EN(PHI0_out), .in(not_22_out), .out(d_latch_26_out));  // open: out_2
  D_LATCH d_latch_27 (.EN(PHI0_out), .in(nand_17_out), .out(d_latch_27_out));  // open: out_2
  not not_60 (not_60_out, nC_OUT);
  nor nor_65 (nor_65_out, d_latch_8_out, not_58_out);
  not not_61 (not_61_out, D48);
  not not_62 (not_62_out, PHI0_out);
  nor nor_66 (nor_66_out, d_latch_21_out, nready);
  nor nor_67 (nor_67_out, nor_21_out, SYNC, D80, D56, nor_55_out);
  and and_18 (and_18_out, nor_61_out, nand_24_out);
  D_LATCH d_latch_28 (.EN(PHI0_out), .in(nor_68_out), .out(d_latch_28_out));  // open: out_2
  nor nor_68 (nor_68_out, D100, D98, d_latch_51_out_2, nor_27_out, not_96_out, nand_29_out);
  nor nor_69 (nor_69_out, nready, d_latch_2_out_2, and_9_out, d_latch_22_out);
  D_LATCH d_latch_29 (.EN(PHI0_out), .in(nor_62_out), .out_2(d_latch_29_out_2));  // open: out
  not not_63 (not_63_out, nor_63_out);
  D_LATCH d_latch_30 (.EN(PHI0_out), .in(and_17_out), .out(d_latch_30_out));  // open: out_2
  not not_64 (not_64_out, nIMPLIED);
  D_LATCH d_latch_31 (.EN(PHI0_out), .in(not_60_out), .out_2(d_latch_31_out_2));  // open: out
  D_LATCH d_latch_32 (.EN(PHI0_out), .in(nor_65_out), .out(d_latch_32_out));  // open: out_2
  nand nand_26 (nand_26_out, D55, d_latch_51_out_2);
  nand nand_27 (nand_27_out, not_61_out, and_14_out);
  D_LATCH d_latch_33 (.EN(not_62_out), .in(nor_66_out), .out_2(d_latch_33_out_2));  // open: out
  nor nor_70 (nor_70_out, nor_67_out, nor_43_out, nor_56_out);
  Transistor #(.\type ("n")) transistor_1 (.in(1'b0), .out(SO), .gate(1'b0));
  nor nor_71 (nor_71_out, nor_69_out, d_latch_29_out_2);
  nor nor_72 (nor_72_out, nor_28_out, nor_10_out, nready);
  and and_19 (and_19_out, nand_25_out, not_63_out);
  xnor xnor_1 (xnor_1_out, not_34_out, ACR);
  and and_20 (and_20_out, xnor_1_out, d_latch_23_out);
  nor nor_73 (nor_73_out, D28, not_95_out, D56, not_27_out);
  nor nor_74 (nor_74_out, d_latch_24_out, d_latch_25_out, d_latch_26_out, d_latch_27_out);
  not not_65 (not_65_out, d_latch_32_out);
  D_LATCH d_latch_34 (.EN(PHI0_out), .in(d_latch_46_out_2), .out(d_latch_34_out));  // open: out_2
  nand nand_28 (nand_28_out, D52, not_66_out);
  not not_66 (not_66_out, nD_OUT);
  not not_67 (not_67_out, nor_52_out);
  nor nor_75 (nor_75_out, nor_52_out, not_15_out);
  not not_68 (not_68_out, nand_26_out);
  nand nand_29 (nand_29_out, d_latch_33_out_2, nor_44_out);
  nor nor_76 (nor_76_out, nor_70_out, D93);
  not not_69 (not_69_out, SO);
  D_LATCH d_latch_35 (.EN(PHI0_out), .in(SYNC), .out_2(d_latch_35_out_2));  // open: out
  and and_21 (and_21_out, nor_71_out, not_70_out);
  not not_70 (not_70_out, BRK6E);
  D_LATCH d_latch_36 (.EN(PHI0_out), .in(nor_72_out), .out(d_latch_36_out));  // open: out_2
  not not_71 (not_71_out, nready);
  not not_72 (not_72_out, PHI0_out);
  nor nor_77 (nor_77_out, d_latch_30_out, nready, not_64_out);
  not not_73 (not_73_out, PHI0_out);
  not not_74 (not_74_out, PHI0_out);
  nor nor_78 (nor_78_out, nready, nor_73_out);
  D_LATCH d_latch_37 (.EN(PHI0_out), .in(not_26_out), .out_2(d_latch_37_out_2));  // open: out
  nand nand_30 (nand_30_out, d_latch_32_out, d_latch_31_out_2);
  nand nand_31 (nand_31_out, not_65_out, d_latch_34_out);
  nand nand_32 (nand_32_out, D51, not_75_out);
  not not_75 (not_75_out, nD_OUT);
  nor nor_79 (nor_79_out, D51, nand_28_out);
  nor nor_80 (nor_80_out, nor_75_out, D67, not_68_out, SYNC, D80, nand_27_out);
  nor nor_81 (nor_81_out, nor_21_out, not_56_out);
  nor nor_82 (nor_82_out, nor_81_out, and_1_out);
  D_LATCH d_latch_38 (.EN(not_76_out), .in(not_69_out), .out_2(d_latch_38_out_2));  // open: out
  not not_76 (not_76_out, PHI0_out);
  nor nor_83 (FETCH, d_latch_35_out_2, nready);
  D_LATCH d_latch_39 (.EN(not_77_out), .in(nor_34_out), .out_2(d_latch_39_out_2));  // open: out
  not not_77 (not_77_out, PHI0_out);
  not not_78 (not_78_out, PHI0_out);
  D_LATCH d_latch_40 (.EN(not_78_out), .in(and_21_out), .out_2(d_latch_40_out_2));  // open: out
  nand nand_33 (nand_33_out, d_latch_50_out, nready);
  not not_79 (not_79_out, d_latch_36_out);
  nand nand_34 (nand_34_out, d_latch_51_out_2, not_71_out);
  nand nand_35 (nand_35_out, and_19_out, D80);
  not not_80 (not_80_out, not_56_out);
  D_LATCH d_latch_41 (.EN(not_72_out), .in(nor_77_out), .out(d_latch_41_out));  // open: out_2
  D_LATCH d_latch_42 (.EN(not_73_out), .in(B_OUT), .out(d_latch_42_out));  // open: out_2
  D_LATCH d_latch_43 (.EN(not_74_out), .in(and_20_out), .out(d_latch_43_out));  // open: out_2
  nor nor_84 (nor_84_out, nor_78_out, nor_64_out);
  not not_81 (not_81_out, not_82_out);
  not not_82 (not_82_out, D93);
  nor nor_85 (nor_85_out, not_22_out, D51, D56);
  not not_83 (not_83_out, nready);
  not not_84 (not_84_out, not_83_out);
  not not_85 (not_85_out, PHI0_out);
  not not_86 (not_86_out, PHI0_out);
  and and_22 (and_22_out, nand_30_out, nand_31_out);
  not not_87 (not_87_out, nor_79_out);
  nand nand_36 (_0_IR, B_OUT, FETCH);
  not not_88 (not_88_out, PHI0_out);
  buf buffer_2 (RW, d_latch_39_out_2);
  not not_89 (not_89_out, PHI0_out);
  and and_23 (and_23_out, nand_33_out, not_79_out);
  D_LATCH d_latch_44 (.EN(PHI0_out), .in(nand_34_out), .out_2(d_latch_44_out_2));  // open: out
  nand nand_37 (nand_37_out, not_56_out, nready);
  and and_24 (and_24_out, nand_35_out, not_80_out);
  or or_3 (or_3_out, nor_84_out, not_81_out);
  or or_4 (or_4_out, nor_85_out, not_84_out);
  nor nor_86 (nor_86_out, not_15_out, not_12_out, not_13_out, not_26_out);
  D_LATCH d_latch_45 (.EN(not_85_out), .in(d_latch_37_out_2), .out(d_latch_45_out));  // open: out_2
  not not_90 (not_90_out, D27);
  D_LATCH d_latch_46 (.EN(not_86_out), .in(and_22_out), .out_2(d_latch_46_out_2));  // open: out
  D_LATCH d_latch_47 (.EN(PHI0_out), .in(nand_32_out), .out_2(d_latch_47_out_2));  // open: out
  D_LATCH d_latch_48 (.EN(PHI0_out), .in(not_87_out), .out_2(d_latch_48_out_2));  // open: out
  nor nor_87 (nor_87_out, nand_19_out, D93);
  D_LATCH d_latch_49 (.EN(PHI0_out), .in(d_latch_38_out_2), .out_2(d_latch_49_out_2));  // open: out
  not not_91 (not_91_out, PHI0_out);
  not not_92 (RD, nor_88_out);
  nor nor_88 (nor_88_out, not_88_out, d_latch_39_out_2);
  D_LATCH d_latch_50 (.EN(PHI0_out), .in(d_latch_51_out_2), .out(d_latch_50_out));  // open: out_2
  D_LATCH d_latch_51 (.EN(not_89_out), .in(and_23_out), .out_2(d_latch_51_out_2));  // open: out
  not not_93 (not_93_out, PHI0_out);
  or or_5 (or_5_out, and_24_out, nready);
  or or_6 (or_6_out, d_latch_41_out, d_latch_43_out);
  and and_25 (and_25_out, or_3_out, not_94_out);
  not not_94 (not_94_out, _0_ADL0);
  nor nor_89 (nor_89_out, d_latch_45_out, not_90_out, d_latch_46_out_2);
  nor nor_90 (nor_90_out, not_96_out, nor_40_out, nand_19_out, SYNC, D56);
  nor nor_91 (nor_91_out, D84, nor_21_out, D93, SYNC, D80, not_56_out);
  not not_95 (not_95_out, nor_91_out);
  nor nor_92 (nor_92_out, D102, d_latch_51_out_2, not_46_out, nor_82_out, D80);
  D_LATCH d_latch_52 (.EN(not_91_out), .in(d_latch_49_out_2), .out(d_latch_52_out));  // open: out_2
  D_LATCH d_latch_53 (.EN(not_93_out), .in(d_latch_44_out_2), .out_2(d_latch_53_out_2));  // open: out
  not not_96 (not_96_out, d_latch_53_out_2);
  and and_26 (and_26_out, nand_37_out, or_5_out);
  not not_97 (_1_PC, and_27_out);
  and and_27 (and_27_out, d_latch_42_out, or_6_out);
  not not_98 (not_98_out, nor_50_out);
  nand nand_38 (nand_38_out, or_4_out, and_6_out);
  not not_99 (not_99_out, nor_42_out);
  D_LATCH d_latch_54 (.EN(PHI0_out), .in(not_15_out), .out_2(d_latch_54_out_2));  // open: out
  D_LATCH d_latch_55 (.EN(PHI0_out), .in(not_12_out), .out_2(d_latch_55_out_2));  // open: out
  D_LATCH d_latch_56 (.EN(PHI0_out), .in(not_13_out), .out_2(d_latch_56_out_2));  // open: out
  D_LATCH d_latch_57 (.EN(PHI0_out), .in(not_26_out), .out_2(d_latch_57_out_2));  // open: out
  D_LATCH d_latch_58 (.EN(PHI0_out), .in(nor_86_out), .out_2(d_latch_58_out_2));  // open: out
  nor nor_93 (nor_93_out, nor_89_out, nor_90_out);
  nor nor_94 (nor_94_out, nand_19_out, nor_22_out);
  not not_100 (not_100_out, and_18_out);
  nor nor_95 (nor_95_out, nor_56_out, not_27_out);
  nor nor_96 (nor_96_out, ACR_C, D109, not_67_out);
  not not_101 (not_101_out, D110);
  not not_102 (not_102_out, D108);
  not not_103 (not_103_out, D120);
  not not_104 (not_104_out, D127);
  nor nor_97 (nor_97_out, d_latch_52_out, d_latch_38_out_2);
  D_LATCH d_latch_59 (.EN(PHI0_out), .in(SYNC), .out(d_latch_59_out));  // open: out_2
  D_LATCH d_latch_60 (.EN(PHI0_out), .in(and_26_out), .out(d_latch_60_out));  // open: out_2
  D_LATCH d_latch_61 (.EN(PHI0_out), .in(RESP), .out(d_latch_61_out));  // open: out_2
  not not_105 (not_105_out, PHI0_out);
  not not_106 (not_106_out, nready);
  not not_107 (not_107_out, PHI0_out);
  not not_108 (not_108_out, PHI0_out);
  not not_109 (not_109_out, PHI0_out);
  not not_110 (not_110_out, PHI0_out);
  not not_111 (not_111_out, PHI0_out);
  not not_112 (not_112_out, PHI0_out);
  not not_113 (not_113_out, PHI0_out);
  not not_114 (not_114_out, nor_94_out);
  not not_115 (not_115_out, PHI0_out);
  not not_116 (not_116_out, nready);
  nor nor_98 (nor_98_out, not_26_out, DB_P);
  nand nand_39 (nand_39_out, d_latch_117_out, nready);
  not not_117 (not_117_out, d_latch_59_out);
  or or_7 (or_7_out, not_117_out, nready);
  nand nand_40 (nand_40_out, d_latch_119_out, nready);
  or or_8 (or_8_out, not_146_out, nready);
  nand nand_41 (nand_41_out, d_latch_121_out, nready);
  or or_9 (or_9_out, not_147_out, nready);
  nand nand_42 (nand_42_out, d_latch_123_out, nready);
  or or_10 (or_10_out, not_148_out, nready);
  nor nor_99 (nor_99_out, d_latch_60_out, d_latch_61_out);
  D_LATCH d_latch_62 (.EN(not_105_out), .in(not_106_out), .out(d_latch_62_out));  // open: out_2
  D_LATCH d_latch_63 (.EN(PHI0_out), .in(and_25_out), .out_2(d_latch_63_out_2));  // open: out
  buf buffer_3 (ADH_ABH, d_latch_63_out_2);
  D_LATCH d_latch_64 (.EN(PHI0_out), .in(nand_23_out), .out_2(d_latch_64_out_2));  // open: out
  buf buffer_4 (ADL_ABL, d_latch_64_out_2);
  D_LATCH d_latch_65 (.EN(PHI0_out), .in(and_10_out), .out_2(d_latch_65_out_2));  // open: out
  buf buffer_5 (buffer_5_out, d_latch_65_out_2);
  D_LATCH d_latch_66 (.EN(PHI0_out), .in(and_11_out), .out_2(d_latch_66_out_2));  // open: out
  buf buffer_6 (buffer_6_out, d_latch_66_out_2);
  D_LATCH d_latch_67 (.EN(PHI0_out), .in(nor_2_out), .out_2(d_latch_67_out_2));  // open: out
  buf buffer_7 (buffer_7_out, d_latch_67_out_2);
  D_LATCH d_latch_68 (.EN(PHI0_out), .in(nor_1_out), .out_2(d_latch_68_out_2));  // open: out
  buf buffer_8 (buffer_8_out, d_latch_68_out_2);
  D_LATCH d_latch_69 (.EN(PHI0_out), .in(not_2_out), .out_2(d_latch_69_out_2));  // open: out
  buf buffer_9 (S_SB, d_latch_69_out_2);
  D_LATCH d_latch_70 (.EN(PHI0_out), .in(and_15_out), .out_2(d_latch_70_out_2));  // open: out
  buf buffer_10 (S_ADL, d_latch_70_out_2);
  D_LATCH d_latch_71 (.EN(PHI0_out), .in(nor_50_out), .out_2(d_latch_71_out_2));  // open: out
  buf buffer_11 (buffer_11_out, d_latch_71_out_2);
  D_LATCH d_latch_72 (.EN(PHI0_out), .in(not_98_out), .out_2(d_latch_72_out_2));  // open: out
  buf buffer_12 (buffer_12_out, d_latch_72_out_2);
  D_LATCH d_latch_73 (.EN(PHI0_out), .in(or_4_out), .out_2(d_latch_73_out_2));  // open: out
  buf buffer_13 (buffer_13_out, d_latch_73_out_2);
  D_LATCH d_latch_74 (.EN(PHI0_out), .in(nand_38_out), .out_2(d_latch_74_out_2));  // open: out
  buf buffer_14 (buffer_14_out, d_latch_74_out_2);
  D_LATCH d_latch_75 (.EN(PHI0_out), .in(nor_42_out), .out_2(d_latch_75_out_2));  // open: out
  buf buffer_15 (buffer_15_out, d_latch_75_out_2);
  D_LATCH d_latch_76 (.EN(PHI0_out), .in(not_99_out), .out_2(d_latch_76_out_2));  // open: out
  buf buffer_16 (buffer_16_out, d_latch_76_out_2);
  D_LATCH d_latch_77 (.EN(PHI0_out), .in(and_6_out), .out_2(d_latch_77_out_2));  // open: out
  buf buffer_17 (buffer_17_out, d_latch_77_out_2);
  D_LATCH d_latch_78 (.EN(not_107_out), .in(d_latch_54_out_2), .out_2(d_latch_78_out_2));  // open: out
  buf buffer_18 (ANDS, d_latch_78_out_2);
  D_LATCH d_latch_79 (.EN(not_108_out), .in(d_latch_55_out_2), .out_2(d_latch_79_out_2));  // open: out
  buf buffer_19 (EORS, d_latch_79_out_2);
  D_LATCH d_latch_80 (.EN(not_109_out), .in(d_latch_56_out_2), .out_2(d_latch_80_out_2));  // open: out
  buf buffer_20 (ORS, d_latch_80_out_2);
  D_LATCH d_latch_81 (.EN(not_110_out), .in(nor_74_out), .out_2(d_latch_81_out_2));  // open: out
  not not_118 (nACIN, d_latch_81_out_2);
  D_LATCH d_latch_82 (.EN(not_111_out), .in(d_latch_57_out_2), .out_2(d_latch_82_out_2));  // open: out
  buf buffer_21 (SRS, d_latch_82_out_2);
  D_LATCH d_latch_83 (.EN(not_112_out), .in(d_latch_58_out_2), .out_2(d_latch_83_out_2));  // open: out
  buf buffer_22 (SUMS, d_latch_83_out_2);
  D_LATCH d_latch_84 (.EN(not_113_out), .in(d_latch_47_out_2), .out_2(d_latch_84_out_2));  // open: out
  buf buffer_23 (nDAA, d_latch_84_out_2);
  D_LATCH d_latch_85 (.EN(PHI0_out), .in(nor_93_out), .out_2(d_latch_85_out_2));  // open: out
  buf buffer_24 (ADD_SB7, d_latch_85_out_2);
  D_LATCH d_latch_86 (.EN(PHI0_out), .in(nor_90_out), .out_2(d_latch_86_out_2));  // open: out
  buf buffer_25 (ADD_SB06, d_latch_86_out_2);
  D_LATCH d_latch_87 (.EN(PHI0_out), .in(not_114_out), .out_2(d_latch_87_out_2));  // open: out
  buf buffer_26 (ADD_ADL, d_latch_87_out_2);
  D_LATCH d_latch_88 (.EN(not_115_out), .in(d_latch_48_out_2), .out_2(nDSA));  // open: out
  D_LATCH d_latch_89 (.EN(PHI0_out), .in(nor_20_out), .out_2(_0_ADH0));  // open: out
  D_LATCH d_latch_90 (.EN(PHI0_out), .in(nor_80_out), .out_2(d_latch_90_out_2));  // open: out
  buf buffer_27 (SB_DB, d_latch_90_out_2);
  D_LATCH d_latch_91 (.EN(PHI0_out), .in(nor_19_out), .out_2(d_latch_91_out_2));  // open: out
  buf buffer_28 (buffer_28_out, d_latch_91_out_2);
  D_LATCH d_latch_92 (.EN(PHI0_out), .in(nor_87_out), .out_2(d_latch_92_out_2));  // open: out
  buf buffer_29 (SB_ADH, d_latch_92_out_2);
  D_LATCH d_latch_93 (.EN(PHI0_out), .in(nor_31_out), .out_2(d_latch_93_out_2));  // open: out
  buf buffer_30 (_0_ADH17, d_latch_93_out_2);
  D_LATCH d_latch_94 (.EN(PHI0_out), .in(and_8_out), .out_2(d_latch_94_out_2));  // open: out
  buf buffer_31 (buffer_31_out, d_latch_94_out_2);
  D_LATCH d_latch_95 (.EN(PHI0_out), .in(and_16_out), .out_2(d_latch_95_out_2));  // open: out
  buf buffer_32 (buffer_32_out, d_latch_95_out_2);
  D_LATCH d_latch_96 (.EN(PHI0_out), .in(nor_91_out), .out_2(d_latch_96_out_2));  // open: out
  buf buffer_33 (buffer_33_out, d_latch_96_out_2);
  D_LATCH d_latch_97 (.EN(PHI0_out), .in(not_95_out), .out_2(d_latch_97_out_2));  // open: out
  buf buffer_34 (buffer_34_out, d_latch_97_out_2);
  D_LATCH d_latch_98 (.EN(PHI0_out), .in(nor_44_out), .out_2(d_latch_98_out_2));  // open: out
  buf buffer_35 (PCH_DB, d_latch_98_out_2);
  D_LATCH d_latch_99 (.EN(PHI0_out), .in(d_latch_33_out_2), .out_2(d_latch_99_out_2));  // open: out
  buf buffer_36 (PCL_DB, d_latch_99_out_2);
  D_LATCH d_latch_100 (.EN(PHI0_out), .in(nor_76_out), .out_2(d_latch_100_out_2));  // open: out
  buf buffer_37 (PCH_ADH, d_latch_100_out_2);
  D_LATCH d_latch_101 (.EN(PHI0_out), .in(not_100_out), .out_2(d_latch_101_out_2));  // open: out
  buf buffer_38 (buffer_38_out, d_latch_101_out_2);
  D_LATCH d_latch_102 (.EN(PHI0_out), .in(nor_67_out), .out_2(d_latch_102_out_2));  // open: out
  buf buffer_39 (PCL_ADL, d_latch_102_out_2);
  D_LATCH d_latch_103 (.EN(PHI0_out), .in(and_18_out), .out_2(d_latch_103_out_2));  // open: out
  buf buffer_40 (buffer_40_out, d_latch_103_out_2);
  D_LATCH d_latch_104 (.EN(PHI0_out), .in(nor_20_out), .out_2(d_latch_104_out_2));  // open: out
  buf buffer_41 (DL_ADL, d_latch_104_out_2);
  D_LATCH d_latch_105 (.EN(PHI0_out), .in(nor_95_out), .out_2(d_latch_105_out_2));  // open: out
  buf buffer_42 (DL_ADH, d_latch_105_out_2);
  D_LATCH d_latch_106 (.EN(PHI0_out), .in(nor_92_out), .out_2(d_latch_106_out_2));  // open: out
  buf buffer_43 (DL_DB, d_latch_106_out_2);
  D_LATCH d_latch_107 (.EN(PHI0_out), .in(nor_26_out), .out_2(P_DB));  // open: out
  D_LATCH d_latch_108 (.EN(PHI0_out), .in(and_12_out), .out_2(ACR_C));  // open: out
  D_LATCH d_latch_109 (.EN(PHI0_out), .in(D112), .out(AVR_V));  // open: out_2
  D_LATCH d_latch_110 (.EN(PHI0_out), .in(nor_96_out), .out(d_latch_110_out), .out_2(DBZ_Z));
  nand nand_43 (nand_43_out, d_latch_11_out, d_latch_110_out);
  and and_28 (DB_N, nand_43_out, not_119_out);
  not not_119 (not_119_out, d_latch_17_out);
  and and_29 (DB_P, d_latch_11_out, not_116_out);
  D_LATCH d_latch_111 (.EN(PHI0_out), .in(nor_98_out), .out_2(DB_C));  // open: out
  nand nand_44 (DB_V, d_latch_10_out, d_latch_11_out);
  D_LATCH d_latch_112 (.EN(PHI0_out), .in(not_101_out), .out_2(IR5_C));  // open: out
  D_LATCH d_latch_113 (.EN(PHI0_out), .in(not_102_out), .out_2(IR5_I));  // open: out
  D_LATCH d_latch_114 (.EN(PHI0_out), .in(not_103_out), .out_2(IR5_D));  // open: out
  D_LATCH d_latch_115 (.EN(PHI0_out), .in(not_104_out), .out_2(_0_V));  // open: out
  D_LATCH d_latch_116 (.EN(PHI0_out), .in(nor_97_out), .out(_1_V));  // open: out_2
  nor nor_100 (nor_100_out, d_latch_40_out_2, d_latch_118_out);
  and and_30 (and_30_out, nand_39_out, or_7_out);
  nor nor_101 (nor_101_out, d_latch_40_out_2, d_latch_120_out);
  and and_31 (and_31_out, nand_40_out, or_8_out);
  nor nor_102 (nor_102_out, d_latch_40_out_2, d_latch_122_out);
  and and_32 (and_32_out, nand_41_out, or_9_out);
  nor nor_103 (nor_103_out, d_latch_40_out_2, d_latch_124_out);
  and and_33 (and_33_out, nand_42_out, or_10_out);
  not not_120 (not_120_out, nor_28_out);
  nor nor_104 (nor_104_out, RESP, d_latch_62_out, d_latch_126_out);
  nor nor_105 (nor_105_out, d_latch_125_out, and_20_out);
  nor nor_106 (nor_106_out, nready, nor_105_out);
  not not_121 (not_121_out, PHI0_out);
  and and_34 (Y_SB, not_121_out, buffer_5_out);
  not not_122 (not_122_out, PHI0_out);
  and and_35 (X_SB, not_122_out, buffer_6_out);
  not not_123 (not_123_out, PHI0_out);
  and and_36 (SB_Y, not_123_out, buffer_7_out);
  not not_124 (not_124_out, PHI0_out);
  and and_37 (SB_X, not_124_out, buffer_8_out);
  not not_125 (not_125_out, PHI0_out);
  and and_38 (SB_S, not_125_out, buffer_11_out);
  not not_126 (not_126_out, PHI0_out);
  and and_39 (S_S, not_126_out, buffer_12_out);
  not not_127 (not_127_out, PHI0_out);
  and and_40 (NDB_ADD, not_127_out, buffer_13_out);
  not not_128 (not_128_out, PHI0_out);
  and and_41 (DB_ADD, not_128_out, buffer_14_out);
  not not_129 (not_129_out, PHI0_out);
  and and_42 (_0_ADD, not_129_out, buffer_15_out);
  not not_130 (not_130_out, PHI0_out);
  and and_43 (SB_ADD, not_130_out, buffer_16_out);
  not not_131 (not_131_out, PHI0_out);
  and and_44 (ADL_ADD, not_131_out, buffer_17_out);
  not not_132 (not_132_out, PHI0_out);
  and and_45 (SB_AC, not_132_out, buffer_28_out);
  not not_133 (not_133_out, PHI0_out);
  and and_46 (AC_SB, not_133_out, buffer_31_out);
  not not_134 (not_134_out, PHI0_out);
  and and_47 (AC_DB, not_134_out, buffer_32_out);
  not not_135 (not_135_out, PHI0_out);
  and and_48 (ADH_PCH, not_135_out, buffer_33_out);
  not not_136 (not_136_out, PHI0_out);
  and and_49 (PCH_PCH, not_136_out, buffer_34_out);
  not not_137 (not_137_out, PHI0_out);
  and and_50 (PCL_PCL, not_137_out, buffer_38_out);
  not not_138 (not_138_out, PHI0_out);
  and and_51 (ADL_PCL, not_138_out, buffer_40_out);
  not not_139 (not_139_out, PHI0_out);
  not not_140 (not_140_out, PHI0_out);
  not not_141 (not_141_out, PHI0_out);
  not not_142 (not_142_out, PHI0_out);
  not not_143 (not_143_out, nor_5_out);
  nor nor_107 (nor_107_out, nor_10_out, D96, not_120_out);
  not not_144 (not_144_out, PHI0_out);
  not not_145 (not_145_out, PHI0_out);
  nor nor_108 (nor_108_out, nor_99_out, nor_106_out);
  not not_146 (not_146_out, d_latch_117_out);
  D_LATCH d_latch_117 (.EN(PHI0_out), .in(nor_100_out), .out(d_latch_117_out));  // open: out_2
  D_LATCH d_latch_118 (.EN(not_139_out), .in(and_30_out), .out(d_latch_118_out));  // open: out_2
  not not_147 (not_147_out, d_latch_119_out);
  D_LATCH d_latch_119 (.EN(PHI0_out), .in(nor_101_out), .out(d_latch_119_out));  // open: out_2
  D_LATCH d_latch_120 (.EN(not_140_out), .in(and_31_out), .out(d_latch_120_out));  // open: out_2
  not not_148 (not_148_out, d_latch_121_out);
  D_LATCH d_latch_121 (.EN(PHI0_out), .in(nor_102_out), .out(d_latch_121_out));  // open: out_2
  D_LATCH d_latch_122 (.EN(not_141_out), .in(and_32_out), .out(d_latch_122_out));  // open: out_2
  D_LATCH d_latch_123 (.EN(PHI0_out), .in(nor_103_out), .out(d_latch_123_out));  // open: out_2
  D_LATCH d_latch_124 (.EN(not_142_out), .in(and_33_out), .out(d_latch_124_out));  // open: out_2
  nor nor_109 (nor_109_out, not_143_out, not_96_out, D93, nor_107_out);
  D_LATCH d_latch_125 (.EN(PHI0_out), .in(nor_104_out), .out(d_latch_125_out));  // open: out_2
  D_LATCH d_latch_126 (.EN(not_144_out), .in(nor_105_out), .out(d_latch_126_out));  // open: out_2
  D_LATCH d_latch_127 (.EN(not_145_out), .in(nor_108_out), .out_2(SYNC));  // open: out
  not not_149 (not_149_out, nor_108_out);
  not not_150 (nT2, nor_100_out);
  not not_151 (nT3, nor_101_out);
  not not_152 (nT4, nor_102_out);
  not not_153 (nT5, nor_103_out);

  assign BR2 = D80;
  assign BRK5 = D22;

  // Notes on the sheet:
  //   Flags
  //   From interrupt control
  //   ACR
  //   #S/SB
  //   RTI/5
  //   T2
  //   STK2
  //   JSR2
  //   SBC0
  //   BR3
  //   JSR/5
  //   RTS/5
  //   RTI/5
  //   BR3
  //   Push/pull
  //   DB7
  //   BR2
  //   #SB/X
  //   #SB/Y
  //   /ready
  //   RET
  //   BRFW
  //   T5
  //   STA
  //   BR2
  //   CSI
  //   BIT1
  //   BIT0
  //   TRESX
  //   /TWOCYCLE
  //   TRES1
  //   STOR
  //   STOR
  //   SBXY
  //   /ready
  //   EORS
  //   /ready
  //   T5
  //   T0
  //   T5
  //   /C_OUT
  //   RDY
  //   Push/pull
  //   RTS/5
  //   JMP/4
  //   AVR/V
  //   CSD
  //   /IR6
  //   /MemOP
  //   /IR7
  //   CLV
  //   IMPL
  //   BRK5
  //   NotReadyPhi1
  //   ORS
  //   #DL/ADL
  //   #SB/AC
  //   #DL/ADL
  //   ABS/2
  //   NOADL
  //   /POUT
  //   STOR
  //   /STORE
  //   /SHIFT
  //   /PIN
  //   RDY
  //   /STORE
  //   /SHIFT
  //   TXS
  //   /ready
  //   BRK6E
  //   JSR2
  //   BRK6E
  //   JSR2
  //   ANDS
  //   Ready delay
  //   SRS
  //   IND
  //   JB
  //   T6
  //   DORES
  //   /ready
  //   ACRL2
  //   ACRL1
  //   /ready
  //   STOR
  //   STOR
  //   JSR2
  //   #ADL/ADD
  //   #0/ADH17
  //   #AC/SB
  //   REST
  //   BRFW
  //   #Y/SB
  //   #X/SB
  //   STK2
  //   RET
  //   INC_SB
  //   JB
  //   NotReadyPhi1
  //   T0
  //   WR
  //   BR2
  //   BR3
  //   STXY
  //   STKOP
  //   SB/ADD
  //   to DL/DB
  //   CSET
  //   SBXY
  //   T6
  //   ANDS
  //   /ready
  //   T5
  //   T6
  //   STA
  //   STOR
  //   #PCH/DB
  //   JB
  //   /ARIT
  //   /ready
  //   /ready
  //   ENDX
  //   /IR5
  //   BR2
  //   /BRTAKEN
  //   #ADL/PCL
  //   BR3
  //   NotReadyPhi1
  //   ACRL2
  //   #S/ADL
  //   #SB/S
  //   CSET
  //   PGX
  //   BR0
  //   BR2
  //   DL/PCH
  //   T0
  //   RTS/5
  //   BR3
  //   NotReadyPhi1
  //   STOR
  //   T6
  //   PC/DB
  //   /ready
  //   ACRL1
  //   91/92
  //   RESP
  //   ENDS
  //   T0
  //   #SB/ADH
  //   /C_OUT
  //   NotReadyPhi1
  //   SRS
  //   /ready
  //   ABS/2
  //   JSR/5
  //   T1
  //   T5
  //   /T0X
  //   /T1X
  //   /IMPLIED
  //   BRFW
  //   ACR
  //   T5
  //   #ADL/ABL
  //   JSR2
  //   STXY
  //   #AC/DB
  //   #PCL/ADL
  //   BR0
  //   /SHIFT
  //   /MemOP
  //   /ready
  //   /ready
  //   T2
  //   #PCH/PCH
  //   JSR/5
  //   IND
  //   /D_OUT
  //   ANDS
  //   BR2
  //   JSXY
  //   #PCL/DB
  //   BR3
  //   #ADL/PCL
  //   SO
  //   T1
  //   BRK6E
  //   /BRTAKEN
  //   SBC0
  //   /ACIN
  //   SRS
  //   SBC0
  //   /D_OUT
  //   SBC0
  //   ZTST
  //   T1
  //   PC/DB
  //   ABS/2
  //   T0
  //   IMPL
  //   B_OUT
  //   /ready
  //   TRESX
  //   /ready
  //   /ready
  //   T0
  //   /ready
  //   /BRTAKEN
  //   BR2
  //   T0
  //   /ready
  //   B_OUT
  //   /ready
  //   BR3
  //   JSR/5
  //   /ready
  //   #ADL/ABL
  //   STKOP
  //   PGX
  //   #PCH/ADH
  //   c
  //   a
  //   b
  //   ROR
  //   T6
  //   T1
  //   #SB/DB
  //   T1
  //   T0
  //   BR2
  //   PGX
  //   BR3
  //   T5
  //   ZTST
  //   0/IR
  //   FETCH
  //   TRES2
  //   0/ADL0
  //   #NDB/ADD
  //   #ADL/ABL
  //   JSR/5
  //   #SB/ADH
  //   JMP/4
  //   BR2
  //   R/W
  //   RESP
  //   #ADL/ADD
  //   #ADD/SB7
  //   #ADD/SB06
  //   PGX
  //   NOADL
  //   #ADD/SB06
  //   #ADH/PCH
  //   DL/PCH
  //   IND
  //   #DL/DB
  //   T1
  //   T5
  //   T6
  //   /ACIN
  //   #PCH/PCH
  //   /ready
  //   SRS
  //   TRES2
  //   /ready
  //   /ready
  //   1/PC
  //   PHI0
  //   ENDS
  //   ENDS
  //   /ready
  //   TRES2
  //   TRES2
  //   TRES2
  //   /MemOP
  //   /SHIFT
  //   RESP
  //   To interrupt control
  //   T6
  //   BR3
  //   ENDX
  //   T1
  //   TRES1
  //   /T2
  //   /T3
  //   /T4
  //   /T5
endmodule

module D_LATCH (
  input  EN,
  input  in,
  output out,
  output out_2
);

  D_Flip_Flop d_ff_1 (.clk(EN), .D(in), .Q(out), .Qn(out_2));  // open: preset, en, reset
endmodule
