// Logisim project 6502.circ as structural Verilog: 49 circuits, main circuit BogusSystem
module BogusSystem (
  input  RDY,
  input  SO,
  input  nNMI,
  input  nIRQ,
  input  nRES
);

  wire n6502_1_phi2, n6502_1_r_w, n6502_1_sync, not_1_out, not_2_out, PHI0_out;
  wire [7:0] n6502_1_d0_2, ram_1_data;
  wire [15:0] n6502_1_a0;

  Clock PHI0 (.out(PHI0_out));
  _6502 u_6502_1 (
    .SYNC(n6502_1_sync), .A0(n6502_1_a0[0]), .A1(n6502_1_a0[1]), .A2(n6502_1_a0[2]), .A3(n6502_1_a0[3]),
    .A4(n6502_1_a0[4]), .A5(n6502_1_a0[5]), .A6(n6502_1_a0[6]), .A7(n6502_1_a0[7]), .D0(ram_1_data[0]),
    .D1(ram_1_data[1]), .D2(ram_1_data[2]), .D3(ram_1_data[3]), .D4(ram_1_data[4]), .D5(ram_1_data[5]),
    .D6(ram_1_data[6]), .D7(ram_1_data[7]), .D0_2(n6502_1_d0_2[0]), .D1_2(n6502_1_d0_2[1]),
    .D2_2(n6502_1_d0_2[2]), .D3_2(n6502_1_d0_2[3]), .D4_2(n6502_1_d0_2[4]), .D5_2(n6502_1_d0_2[5]),
    .D6_2(n6502_1_d0_2[6]), .D7_2(n6502_1_d0_2[7]), .nNMI(nNMI), .nIRQ(nIRQ), .RDY(RDY), .nRES(nRES),
    .PHI2(n6502_1_phi2), .SO(SO), .R_W(n6502_1_r_w), .A8(n6502_1_a0[8]), .A9(n6502_1_a0[9]),
    .A10(n6502_1_a0[10]), .A11(n6502_1_a0[11]), .A12(n6502_1_a0[12]), .A13(n6502_1_a0[13]),
    .A14(n6502_1_a0[14]), .A15(n6502_1_a0[15]), .PHI0(PHI0_out));  // open: PHI1
  Counter #(.width(32), .max('hffffffff)) counter_1 (
    .count(1'b1), .clk(n6502_1_phi2), .clr(not_1_out));  // open: load, D, Q, carry
  not not_1 (not_1_out, nRES);
  not not_2 (not_2_out, n6502_1_r_w);
  Counter #(.width(32), .max('hffffffff)) counter_2 (
    .count(1'b1), .clk(n6502_1_sync), .clr(not_1_out));  // open: load, D, Q, carry
  RAM #(.addrWidth(16), .bus("separate")) ram_1 (
    .addr(n6502_1_a0), .din(n6502_1_d0_2), .data(ram_1_data), .str(not_2_out), .sel(n6502_1_phi2),
    .clk(n6502_1_phi2), .ld(n6502_1_r_w));  // open: clr

  // Notes on the sheet:
  //   CLK Counter
  //   Instr Counter
endmodule

module _6502 (
  input  nNMI,
  input  nIRQ,
  input  RDY,
  input  nRES,
  input  SO,
  input  PHI0,
  input  D0,
  input  D1,
  input  D2,
  input  D3,
  input  D4,
  input  D5,
  input  D6,
  input  D7,
  output PHI1,
  output PHI2,
  output R_W,
  output SYNC,
  output A0,
  output A1,
  output A2,
  output A3,
  output A4,
  output A5,
  output A6,
  output A7,
  output D0_2,
  output D1_2,
  output D2_2,
  output D3_2,
  output D4_2,
  output D5_2,
  output A8,
  output A9,
  output A10,
  output A11,
  output A12,
  output A13,
  output A14,
  output A15,
  output D6_2,
  output D7_2
);

  wire alu_1_acr, alu_1_avr, bus_mux_hack_1_sbdb_clutch, decoder_trans_1__0, decoder_trans_1__1,
       decoder_trans_1__2, decoder_trans_1__3, decoder_trans_1__4, decoder_trans_1__5, decoder_trans_1__6,
       decoder_trans_1__7, decoder_trans_1__8, decoder_trans_1__9, decoder_trans_1__10, decoder_trans_1__11,
       decoder_trans_1__12, decoder_trans_1__13, decoder_trans_1__14, decoder_trans_1__15,
       decoder_trans_1__16, decoder_trans_1__17, decoder_trans_1__18, decoder_trans_1__19,
       decoder_trans_1__20, decoder_trans_1__21, decoder_trans_1__22, decoder_trans_1__23,
       decoder_trans_1__24, decoder_trans_1__25, decoder_trans_1__26, decoder_trans_1__27,
       decoder_trans_1__28, decoder_trans_1__29, decoder_trans_1__30, decoder_trans_1__31,
       decoder_trans_1__32, decoder_trans_1__33, decoder_trans_1__34, decoder_trans_1__35,
       decoder_trans_1__36, decoder_trans_1__37, decoder_trans_1__38, decoder_trans_1__39,
       decoder_trans_1__40, decoder_trans_1__41, decoder_trans_1__42, decoder_trans_1__43,
       decoder_trans_1__44, decoder_trans_1__45, decoder_trans_1__46, decoder_trans_1__47,
       decoder_trans_1__48, decoder_trans_1__49, decoder_trans_1__50, decoder_trans_1__51,
       decoder_trans_1__52, decoder_trans_1__53, decoder_trans_1__54, decoder_trans_1__55,
       decoder_trans_1__56, decoder_trans_1__57, decoder_trans_1__58, decoder_trans_1__59,
       decoder_trans_1__60, decoder_trans_1__61, decoder_trans_1__62, decoder_trans_1__63,
       decoder_trans_1__64, decoder_trans_1__65, decoder_trans_1__66, decoder_trans_1__67,
       decoder_trans_1__68, decoder_trans_1__69, decoder_trans_1__70, decoder_trans_1__71,
       decoder_trans_1__72, decoder_trans_1__73, decoder_trans_1__74, decoder_trans_1__75,
       decoder_trans_1__76, decoder_trans_1__77, decoder_trans_1__78, decoder_trans_1__79,
       decoder_trans_1__80, decoder_trans_1__81, decoder_trans_1__82, decoder_trans_1__83,
       decoder_trans_1__84, decoder_trans_1__85, decoder_trans_1__86, decoder_trans_1__87,
       decoder_trans_1__88, decoder_trans_1__89, decoder_trans_1__90, decoder_trans_1__91,
       decoder_trans_1__92, decoder_trans_1__93, decoder_trans_1__94, decoder_trans_1__95,
       decoder_trans_1__96, decoder_trans_1__97, decoder_trans_1__98, decoder_trans_1__99,
       decoder_trans_1__100, decoder_trans_1__101, decoder_trans_1__102, decoder_trans_1__103,
       decoder_trans_1__104, decoder_trans_1__105, decoder_trans_1__106, decoder_trans_1__107,
       decoder_trans_1__108, decoder_trans_1__109, decoder_trans_1__110, decoder_trans_1__111,
       decoder_trans_1__112, decoder_trans_1__113, decoder_trans_1__114, decoder_trans_1__115,
       decoder_trans_1__116, decoder_trans_1__117, decoder_trans_1__118, decoder_trans_1__119,
       decoder_trans_1__120, decoder_trans_1__121, decoder_trans_1__122, decoder_trans_1__123,
       decoder_trans_1__124, decoder_trans_1__125, decoder_trans_1__126, decoder_trans_1__127,
       decoder_trans_1__128, decoder_trans_1__129, dff_level_1_not_q, dff_level_2_not_q, dff_level_3_q,
       IR_ir0, IR_ir1, IR_ir2, IR_ir3, IR_ir4, IR_ir5, IR_ir6, IR_ir7, irqp_latch_not_q, not_1_out,
       not_2_out, not_3_out, prdy_latch1_not_q, prdy_latch2_not_q, PREDECODE_nimplied, PREDECODE_npd0,
       PREDECODE_npd1, PREDECODE_npd2, PREDECODE_npd3, PREDECODE_npd4, PREDECODE_npd5, PREDECODE_npd6,
       PREDECODE_npd7, PREDECODE_ntwocycle, random_logic_1__0_ir, random_logic_1__0_v, random_logic_1_acr_c,
       random_logic_1_db_c, random_logic_1_db_n, random_logic_1_db_p, random_logic_1_db_v,
       random_logic_1_dbz_z, random_logic_1_ends, random_logic_1_endx, random_logic_1_fetch,
       random_logic_1_ir5_c, random_logic_1_ir5_d, random_logic_1_ir5_i, random_logic_1_nc_out,
       random_logic_1_nd_out, random_logic_1_ni_out, random_logic_1_nn_out, random_logic_1_nt0,
       random_logic_1_nt1x, random_logic_1_nt2, random_logic_1_nt3, random_logic_1_nt4, random_logic_1_nt5,
       random_logic_1_nv_out, random_logic_1_nz_out, random_logic_1_p_db, random_logic_1_t1,
       random_logic_1_tres1, random_logic_1_tres2, random_logic_1_tresx, random_logic_1_wr, resp_latch_not_q;
  wire [1:0] random_logic_1_adh_abh;
  wire [2:0] Dirty, random_logic_1_dl_adl, random_logic_1_nacin;
  wire [4:0] random_logic_1__0_adl0, random_logic_1_sb_adh;
  wire [7:0] alu_1_ac_debug, alu_1_add_debug, alu_1_adh0, alu_1_ai_debug, alu_1_bi_debug,
       const_gen_1_adh_out, const_gen_1_adl_out, dl_1_dl_debug, dl_1_dor_debug, precharge_1_adh_out,
       precharge_1_adl_out, precharge_1_db_out, precharge_1_sb_out, random_logic_1_db0_2,
       random_logic_1_y_sb, regs_1_adl0, regs_1_s_debug, regs_1_sb0_2, regs_1_x_debug, regs_1_y_debug;
  wire [8:0] random_logic_1_adh_pch;
  wire [12:0] random_logic_1_ndb_add;
  wire [15:0] pc_1_pc_debug, pc_1_pcs_debug;

  PRECHARGE precharge_1 (
    .PHI2(PHI2), .SB_In(regs_1_sb0_2), .DB_In(random_logic_1_db0_2), .ADL_In(regs_1_adl0),
    .ADH_In(alu_1_adh0), .SB_Out(precharge_1_sb_out), .DB_Out(precharge_1_db_out),
    .ADL_Out(precharge_1_adl_out), .ADH_Out(precharge_1_adh_out), ._0_ADD(random_logic_1_ndb_add[2]),
    .SB_ADD(random_logic_1_ndb_add[3]));
  buf buffer_1 (SYNC, random_logic_1_t1);
  CONST_GEN const_gen_1 (
    ._0_ADH0(random_logic_1__0_adl0[3]), ._0_ADH17(random_logic_1__0_adl0[4]),
    ._0_ADL0(random_logic_1__0_adl0[0]), ._0_ADL1(random_logic_1__0_adl0[1]),
    ._0_ADL2(random_logic_1__0_adl0[2]), .ADL_In(precharge_1_adl_out), .ADH_In(precharge_1_adh_out),
    .ADL_Out(const_gen_1_adl_out), .ADH_Out(const_gen_1_adh_out));
  DFF_Level dff_level_1 (.EN(PHI2), .D(nNMI), .NOT_Q(dff_level_1_not_q));  // open: Q
  not not_1 (not_1_out, dff_level_1_not_q);
  DECODER_TRANS decoder_trans_1 (
    .nT5(random_logic_1_nt5), .nT4(random_logic_1_nt4), .nT3(random_logic_1_nt3), .nT2(random_logic_1_nt2),
    .IR0(IR_ir0), .IR1(IR_ir1), .IR7(IR_ir7), .IR4(IR_ir4), .IR3(IR_ir3), .IR2(IR_ir2), .IR6(IR_ir6),
    .IR5(IR_ir5), .nT0(random_logic_1_nt0), .nT1X(random_logic_1_nt1x), ._0(decoder_trans_1__0),
    ._1(decoder_trans_1__1), ._2(decoder_trans_1__2), ._3(decoder_trans_1__3), ._4(decoder_trans_1__4),
    ._5(decoder_trans_1__5), ._6(decoder_trans_1__6), ._7(decoder_trans_1__7), ._8(decoder_trans_1__8),
    ._9(decoder_trans_1__9), ._10(decoder_trans_1__10), ._11(decoder_trans_1__11), ._12(decoder_trans_1__12),
    ._13(decoder_trans_1__13), ._14(decoder_trans_1__14), ._15(decoder_trans_1__15),
    ._16(decoder_trans_1__16), ._17(decoder_trans_1__17), ._18(decoder_trans_1__18),
    ._19(decoder_trans_1__19), ._20(decoder_trans_1__20), ._21(decoder_trans_1__21),
    ._22(decoder_trans_1__22), ._23(decoder_trans_1__23), ._24(decoder_trans_1__24),
    ._25(decoder_trans_1__25), ._26(decoder_trans_1__26), ._27(decoder_trans_1__27),
    ._28(decoder_trans_1__28), ._29(decoder_trans_1__29), ._30(decoder_trans_1__30),
    ._31(decoder_trans_1__31), ._32(decoder_trans_1__32), ._33(decoder_trans_1__33),
    ._34(decoder_trans_1__34), ._35(decoder_trans_1__35), ._36(decoder_trans_1__36),
    ._37(decoder_trans_1__37), ._38(decoder_trans_1__38), ._39(decoder_trans_1__39),
    ._40(decoder_trans_1__40), ._41(decoder_trans_1__41), ._42(decoder_trans_1__42),
    ._43(decoder_trans_1__43), ._44(decoder_trans_1__44), ._45(decoder_trans_1__45),
    ._46(decoder_trans_1__46), ._47(decoder_trans_1__47), ._48(decoder_trans_1__48),
    ._49(decoder_trans_1__49), ._50(decoder_trans_1__50), ._51(decoder_trans_1__51),
    ._52(decoder_trans_1__52), ._53(decoder_trans_1__53), ._54(decoder_trans_1__54),
    ._55(decoder_trans_1__55), ._56(decoder_trans_1__56), ._57(decoder_trans_1__57),
    ._58(decoder_trans_1__58), ._59(decoder_trans_1__59), ._60(decoder_trans_1__60),
    ._61(decoder_trans_1__61), ._62(decoder_trans_1__62), ._63(decoder_trans_1__63),
    ._64(decoder_trans_1__64), ._65(decoder_trans_1__65), ._66(decoder_trans_1__66),
    ._67(decoder_trans_1__67), ._68(decoder_trans_1__68), ._69(decoder_trans_1__69),
    ._70(decoder_trans_1__70), ._71(decoder_trans_1__71), ._72(decoder_trans_1__72),
    ._73(decoder_trans_1__73), ._74(decoder_trans_1__74), ._75(decoder_trans_1__75),
    ._76(decoder_trans_1__76), ._77(decoder_trans_1__77), ._78(decoder_trans_1__78),
    ._79(decoder_trans_1__79), ._80(decoder_trans_1__80), ._81(decoder_trans_1__81),
    ._82(decoder_trans_1__82), ._83(decoder_trans_1__83), ._84(decoder_trans_1__84),
    ._85(decoder_trans_1__85), ._86(decoder_trans_1__86), ._87(decoder_trans_1__87),
    ._88(decoder_trans_1__88), ._89(decoder_trans_1__89), ._90(decoder_trans_1__90),
    ._91(decoder_trans_1__91), ._92(decoder_trans_1__92), ._93(decoder_trans_1__93),
    ._94(decoder_trans_1__94), ._95(decoder_trans_1__95), ._96(decoder_trans_1__96),
    ._97(decoder_trans_1__97), ._98(decoder_trans_1__98), ._99(decoder_trans_1__99),
    ._100(decoder_trans_1__100), ._101(decoder_trans_1__101), ._102(decoder_trans_1__102),
    ._103(decoder_trans_1__103), ._104(decoder_trans_1__104), ._105(decoder_trans_1__105),
    ._106(decoder_trans_1__106), ._107(decoder_trans_1__107), ._108(decoder_trans_1__108),
    ._109(decoder_trans_1__109), ._110(decoder_trans_1__110), ._111(decoder_trans_1__111),
    ._112(decoder_trans_1__112), ._113(decoder_trans_1__113), ._114(decoder_trans_1__114),
    ._115(decoder_trans_1__115), ._116(decoder_trans_1__116), ._117(decoder_trans_1__117),
    ._118(decoder_trans_1__118), ._119(decoder_trans_1__119), ._120(decoder_trans_1__120),
    ._121(decoder_trans_1__121), ._122(decoder_trans_1__122), ._123(decoder_trans_1__123),
    ._124(decoder_trans_1__124), ._125(decoder_trans_1__125), ._126(decoder_trans_1__126),
    ._127(decoder_trans_1__127), ._128(decoder_trans_1__128), ._129(decoder_trans_1__129));
  RANDOM_LOGIC random_logic_1 (
    .X0(decoder_trans_1__0), .X1(decoder_trans_1__1), .X2(decoder_trans_1__2), .X3(decoder_trans_1__3),
    .X4(decoder_trans_1__4), .X5(decoder_trans_1__5), .X6(decoder_trans_1__6), .X7(decoder_trans_1__7),
    .X8(decoder_trans_1__8), .X9(decoder_trans_1__9), .X10(decoder_trans_1__10), .X11(decoder_trans_1__11),
    .X12(decoder_trans_1__12), .X13(decoder_trans_1__13), .X14(decoder_trans_1__14),
    .X15(decoder_trans_1__15), .X16(decoder_trans_1__16), .X17(decoder_trans_1__17),
    .X18(decoder_trans_1__18), .X19(decoder_trans_1__19), .X20(decoder_trans_1__20),
    .X21(decoder_trans_1__21), .X22(decoder_trans_1__22), .X23(decoder_trans_1__23),
    .X24(decoder_trans_1__24), .X25(decoder_trans_1__25), .X26(decoder_trans_1__26),
    .X27(decoder_trans_1__27), .X28(decoder_trans_1__28), .X29(decoder_trans_1__29),
    .X30(decoder_trans_1__30), .X31(decoder_trans_1__31), .X32(decoder_trans_1__32),
    .X33(decoder_trans_1__33), .X34(decoder_trans_1__34), .X35(decoder_trans_1__35),
    .X36(decoder_trans_1__36), .X37(decoder_trans_1__37), .X38(decoder_trans_1__38),
    .X39(decoder_trans_1__39), .X40(decoder_trans_1__40), .X41(decoder_trans_1__41),
    .X42(decoder_trans_1__42), .X43(decoder_trans_1__43), .X44(decoder_trans_1__44),
    .X45(decoder_trans_1__45), .X46(decoder_trans_1__46), .X47(decoder_trans_1__47),
    .X48(decoder_trans_1__48), .X49(decoder_trans_1__49), .X50(decoder_trans_1__50),
    .X51(decoder_trans_1__51), .X52(decoder_trans_1__52), .X53(decoder_trans_1__53),
    .X54(decoder_trans_1__54), .X55(decoder_trans_1__55), .X56(decoder_trans_1__56),
    .X57(decoder_trans_1__57), .X58(decoder_trans_1__58), .X59(decoder_trans_1__59),
    .X60(decoder_trans_1__60), .X61(decoder_trans_1__61), .X62(decoder_trans_1__62),
    .X63(decoder_trans_1__63), .X64(decoder_trans_1__64), .X65(decoder_trans_1__65),
    .X66(decoder_trans_1__66), .X67(decoder_trans_1__67), .X68(decoder_trans_1__68),
    .X69(decoder_trans_1__69), .X70(decoder_trans_1__70), .X71(decoder_trans_1__71),
    .X72(decoder_trans_1__72), .X73(decoder_trans_1__73), .X74(decoder_trans_1__74),
    .X75(decoder_trans_1__75), .X76(decoder_trans_1__76), .X77(decoder_trans_1__77),
    .X78(decoder_trans_1__78), .X79(decoder_trans_1__79), .X80(decoder_trans_1__80),
    .X81(decoder_trans_1__81), .X82(decoder_trans_1__82), .X83(decoder_trans_1__83),
    .X84(decoder_trans_1__84), .X85(decoder_trans_1__85), .X86(decoder_trans_1__86),
    .X87(decoder_trans_1__87), .X88(decoder_trans_1__88), .X89(decoder_trans_1__89),
    .X90(decoder_trans_1__90), .X91(decoder_trans_1__91), .X92(decoder_trans_1__92),
    .X93(decoder_trans_1__93), .X94(decoder_trans_1__94), .X95(decoder_trans_1__95),
    .X96(decoder_trans_1__96), .X97(decoder_trans_1__97), .X98(decoder_trans_1__98),
    .X99(decoder_trans_1__99), .X100(decoder_trans_1__100), .X101(decoder_trans_1__101),
    .X102(decoder_trans_1__102), .X103(decoder_trans_1__103), .X104(decoder_trans_1__104),
    .X105(decoder_trans_1__105), .X106(decoder_trans_1__106), .X107(decoder_trans_1__107),
    .X108(decoder_trans_1__108), .X109(decoder_trans_1__109), .X110(decoder_trans_1__110),
    .X111(decoder_trans_1__111), .X112(decoder_trans_1__112), .X113(decoder_trans_1__113),
    .X114(decoder_trans_1__114), .X115(decoder_trans_1__115), .X116(decoder_trans_1__116),
    .X117(decoder_trans_1__117), .X118(decoder_trans_1__118), .X119(decoder_trans_1__119),
    .X120(decoder_trans_1__120), .X121(decoder_trans_1__121), .X122(decoder_trans_1__122),
    .X123(decoder_trans_1__123), .X124(decoder_trans_1__124), .X125(decoder_trans_1__125),
    .X126(decoder_trans_1__126), .X127(decoder_trans_1__127), .X128(decoder_trans_1__128),
    .X129(decoder_trans_1__129), .nNMIP(not_1_out), .nIRQP(irqp_latch_not_q), .RESP(resp_latch_not_q),
    .RDY(RDY), .nT0(random_logic_1_nt0), .nT1X(random_logic_1_nt1x), .nT2(random_logic_1_nt2),
    .nT3(random_logic_1_nt3), .nT4(random_logic_1_nt4), .nT5(random_logic_1_nt5), .PHI1(PHI1), .PHI2(PHI2),
    .nTWOCYCLE(PREDECODE_ntwocycle), .nIMPLIED(PREDECODE_nimplied), .FETCH(random_logic_1_fetch),
    .WR(random_logic_1_wr), .DB0(precharge_1_db_out[0]), .DB1(precharge_1_db_out[1]),
    .DB2(precharge_1_db_out[2]), .DB3(precharge_1_db_out[3]), .DB4(precharge_1_db_out[4]),
    .DB5(precharge_1_db_out[5]), .DB6(precharge_1_db_out[6]), .DB7(precharge_1_db_out[7]), .AVR(alu_1_avr),
    .ADH_ABH(random_logic_1_adh_abh[0]), .ADL_ABL(random_logic_1_adh_abh[1]), .Y_SB(random_logic_1_y_sb[0]),
    .X_SB(random_logic_1_y_sb[2]), ._0_ADL0(random_logic_1__0_adl0[0]), ._0_ADL1(random_logic_1__0_adl0[1]),
    ._0_ADL2(random_logic_1__0_adl0[2]), .SB_Y(random_logic_1_y_sb[1]), .SB_X(random_logic_1_y_sb[3]),
    .S_SB(random_logic_1_y_sb[7]), .S_ADL(random_logic_1_y_sb[4]), .SB_S(random_logic_1_y_sb[6]),
    .S_S(random_logic_1_y_sb[5]), ._0_IR(random_logic_1__0_ir), .NDB_ADD(random_logic_1_ndb_add[0]),
    .DB_ADD(random_logic_1_ndb_add[1]), ._0_ADD(random_logic_1_ndb_add[2]),
    .SB_ADD(random_logic_1_ndb_add[3]), .ADL_ADD(random_logic_1_ndb_add[4]),
    .ANDS(random_logic_1_ndb_add[8]), .EORS(random_logic_1_ndb_add[9]), .ORS(random_logic_1_ndb_add[10]),
    .nACIN(random_logic_1_nacin[0]), .SUMS(random_logic_1_ndb_add[12]), .nDAA(random_logic_1_nacin[1]),
    .ADD_SB7(random_logic_1_ndb_add[6]), .ADD_SB06(random_logic_1_ndb_add[5]),
    .ADD_ADL(random_logic_1_ndb_add[7]), .nDSA(random_logic_1_nacin[2]), .nIR5(not_3_out),
    .SB_AC(random_logic_1_sb_adh[4]), .AC_SB(random_logic_1_sb_adh[3]), .DL_ADH(random_logic_1_dl_adl[2]),
    .DL_DB(random_logic_1_dl_adl[1]), .DL_ADL(random_logic_1_dl_adl[0]),
    ._0_ADH17(random_logic_1__0_adl0[4]), .AC_DB(random_logic_1_sb_adh[2]), .SB_DB(random_logic_1_sb_adh[1]),
    .SB_ADH(random_logic_1_sb_adh[0]), .SO(SO), .SRS(random_logic_1_ndb_add[11]), .ENDX(random_logic_1_endx),
    .ENDS(random_logic_1_ends), .TRES1(random_logic_1_tres1), ._1_PC(random_logic_1_adh_pch[8]),
    .ADL_PCL(random_logic_1_adh_pch[4]), .PCL_PCL(random_logic_1_adh_pch[5]),
    .PCH_ADH(random_logic_1_adh_pch[2]), .PCL_ADL(random_logic_1_adh_pch[6]),
    .PCH_DB(random_logic_1_adh_pch[3]), .PCL_DB(random_logic_1_adh_pch[7]), .P_DB(random_logic_1_p_db),
    .IR5_I(random_logic_1_ir5_i), .IR5_C(random_logic_1_ir5_c), .IR5_D(random_logic_1_ir5_d),
    ._0_V(random_logic_1__0_v), .ACR_C(random_logic_1_acr_c), .DBZ_Z(random_logic_1_dbz_z),
    .DB_N(random_logic_1_db_n), .DB_P(random_logic_1_db_p), .TRESX(random_logic_1_tresx),
    .DB_C(random_logic_1_db_c), .DB_V(random_logic_1_db_v), .ADH_PCH(random_logic_1_adh_pch[0]),
    .PCH_PCH(random_logic_1_adh_pch[1]), .nV_OUT(random_logic_1_nv_out), .nI_OUT(random_logic_1_ni_out),
    .nD_OUT(random_logic_1_nd_out), .nC_OUT(random_logic_1_nc_out), .nN_OUT(random_logic_1_nn_out),
    .nZ_OUT(random_logic_1_nz_out), .ACR(alu_1_acr), .T1(random_logic_1_t1), .DB0_2(random_logic_1_db0_2[0]),
    .DB1_2(random_logic_1_db0_2[1]), .DB2_2(random_logic_1_db0_2[2]), .DB3_2(random_logic_1_db0_2[3]),
    .DB7_2(random_logic_1_db0_2[7]), .DB6_2(random_logic_1_db0_2[6]), .DB5_2(random_logic_1_db0_2[5]),
    .DB4_2(random_logic_1_db0_2[4]), ._0_ADH0(random_logic_1__0_adl0[3]), .nPRDY(prdy_latch2_not_q),
    .TRES2(random_logic_1_tres2));
  ABL abl_1 (
    .PHI1(PHI1), .PHI2(PHI2), .ADL_ABL(random_logic_1_adh_abh[1]), .ADL0(const_gen_1_adl_out[0]),
    .ADL1(const_gen_1_adl_out[1]), .ADL2(const_gen_1_adl_out[2]), .ADL3(const_gen_1_adl_out[3]),
    .ADL4(const_gen_1_adl_out[4]), .ADL5(const_gen_1_adl_out[5]), .ADL6(const_gen_1_adl_out[6]),
    .ADL7(const_gen_1_adl_out[7]), .A0(A0), .A1(A1), .A2(A2), .A3(A3), .A4(A4), .A5(A5), .A6(A6), .A7(A7));
  ABH abh_1 (
    .PHI1(PHI1), .ADH_ABH(random_logic_1_adh_abh[0]), .ADH0(const_gen_1_adh_out[0]),
    .ADH1(const_gen_1_adh_out[1]), .ADH2(const_gen_1_adh_out[2]), .ADH3(const_gen_1_adh_out[3]),
    .ADH4(const_gen_1_adh_out[4]), .ADH5(const_gen_1_adh_out[5]), .ADH6(const_gen_1_adh_out[6]),
    .ADH7(const_gen_1_adh_out[7]), .A8(A8), .A9(A9), .A10(A10), .A11(A11), .A12(A12), .A13(A13), .A14(A14),
    .A15(A15), .PHI2(PHI2));
  DFF_Level dff_level_2 (.EN(PHI2), .D(nIRQ), .NOT_Q(dff_level_2_not_q));  // open: Q
  D_Latch irqp_latch (.EN(PHI1), .D(dff_level_2_not_q), .NOT_Q(irqp_latch_not_q));  // open: Q
  REGS regs_1 (
    .PHI2(PHI2), .Y_SB(random_logic_1_y_sb[0]), .SB_Y(random_logic_1_y_sb[1]), .X_SB(random_logic_1_y_sb[2]),
    .SB_X(random_logic_1_y_sb[3]), .S_ADL(random_logic_1_y_sb[4]), .S_S(random_logic_1_y_sb[5]),
    .SB_S(random_logic_1_y_sb[6]), .S_SB(random_logic_1_y_sb[7]), .SB0(precharge_1_sb_out[0]),
    .SB1(precharge_1_sb_out[1]), .SB2(precharge_1_sb_out[2]), .SB3(precharge_1_sb_out[3]),
    .SB4(precharge_1_sb_out[4]), .SB5(precharge_1_sb_out[5]), .SB6(precharge_1_sb_out[6]),
    .SB7(precharge_1_sb_out[7]), .SB0_2(regs_1_sb0_2[0]), .SB1_2(regs_1_sb0_2[1]), .SB2_2(regs_1_sb0_2[2]),
    .SB3_2(regs_1_sb0_2[3]), .SB4_2(regs_1_sb0_2[4]), .SB5_2(regs_1_sb0_2[5]), .SB6_2(regs_1_sb0_2[6]),
    .SB7_2(regs_1_sb0_2[7]), .ADL0(regs_1_adl0[0]), .ADL1(regs_1_adl0[1]), .ADL2(regs_1_adl0[2]),
    .ADL3(regs_1_adl0[3]), .ADL4(regs_1_adl0[4]), .ADL5(regs_1_adl0[5]), .ADL6(regs_1_adl0[6]),
    .ADL7(regs_1_adl0[7]), .X_Debug(regs_1_x_debug), .Y_Debug(regs_1_y_debug), .S_Debug(regs_1_s_debug));
  Register #(.trigger("high")) X (.D(regs_1_x_debug), .en(1'b1), .clk(1'b1));  // open: Q, clr
  Register #(.trigger("high")) Y (.D(regs_1_y_debug), .en(1'b1), .clk(1'b1));  // open: Q, clr
  Register #(.trigger("high")) S (.D(regs_1_s_debug), .en(1'b1), .clk(1'b1));  // open: Q, clr
  not not_2 (not_2_out, RDY);
  D_Latch prdy_latch1 (.EN(PHI2), .D(not_2_out), .NOT_Q(prdy_latch1_not_q));  // open: Q
  ALU alu_1 (
    .PHI2(PHI2), .NDB_ADD(random_logic_1_ndb_add[0]), .DB_ADD(random_logic_1_ndb_add[1]),
    ._0_ADD(random_logic_1_ndb_add[2]), .SB_ADD(random_logic_1_ndb_add[3]),
    .ADL_ADD(random_logic_1_ndb_add[4]), .ADD_SB06(random_logic_1_ndb_add[5]),
    .ADD_SB7(random_logic_1_ndb_add[6]), .ADD_ADL(random_logic_1_ndb_add[7]),
    .ANDS(random_logic_1_ndb_add[8]), .EORS(random_logic_1_ndb_add[9]), .ORS(random_logic_1_ndb_add[10]),
    .SRS(random_logic_1_ndb_add[11]), .SUMS(random_logic_1_ndb_add[12]), .SB_AC(random_logic_1_sb_adh[4]),
    .AC_SB(random_logic_1_sb_adh[3]), .AC_DB(random_logic_1_sb_adh[2]), .SB_DB(random_logic_1_sb_adh[1]),
    .SB_ADH(random_logic_1_sb_adh[0]), .nACIN(random_logic_1_nacin[0]), .nDAA(random_logic_1_nacin[1]),
    .nDSA(random_logic_1_nacin[2]), .SB0(precharge_1_sb_out[0]), .SB1(precharge_1_sb_out[1]),
    .SB2(precharge_1_sb_out[2]), .SB3(precharge_1_sb_out[3]), .SB4(precharge_1_sb_out[4]),
    .SB5(precharge_1_sb_out[5]), .SB6(precharge_1_sb_out[6]), .SB7(precharge_1_sb_out[7]),
    .DB0(precharge_1_db_out[0]), .DB1(precharge_1_db_out[1]), .DB2(precharge_1_db_out[2]),
    .DB3(precharge_1_db_out[3]), .DB4(precharge_1_db_out[4]), .DB5(precharge_1_db_out[5]),
    .DB6(precharge_1_db_out[6]), .DB7(precharge_1_db_out[7]), .ADL_In(const_gen_1_adl_out), .ACR(alu_1_acr),
    .AVR(alu_1_avr), .SB0_2(regs_1_sb0_2[0]), .SB1_2(regs_1_sb0_2[1]), .SB2_2(regs_1_sb0_2[2]),
    .SB3_2(regs_1_sb0_2[3]), .SB4_2(regs_1_sb0_2[4]), .SB5_2(regs_1_sb0_2[5]), .SB6_2(regs_1_sb0_2[6]),
    .SB7_2(regs_1_sb0_2[7]), .DB0_2(random_logic_1_db0_2[0]), .DB1_2(random_logic_1_db0_2[1]),
    .DB2_2(random_logic_1_db0_2[2]), .DB3_2(random_logic_1_db0_2[3]), .DB4_2(random_logic_1_db0_2[4]),
    .DB5_2(random_logic_1_db0_2[5]), .DB6_2(random_logic_1_db0_2[6]), .DB7_2(random_logic_1_db0_2[7]),
    .ADL0(regs_1_adl0[0]), .ADL1(regs_1_adl0[1]), .ADL2(regs_1_adl0[2]), .ADL3(regs_1_adl0[3]),
    .ADL4(regs_1_adl0[4]), .ADL5(regs_1_adl0[5]), .ADL6(regs_1_adl0[6]), .ADL7(regs_1_adl0[7]),
    .ADH0(alu_1_adh0[0]), .ADH1(alu_1_adh0[1]), .ADH2(alu_1_adh0[2]), .ADH3(alu_1_adh0[3]),
    .ADH4(alu_1_adh0[4]), .ADH5(alu_1_adh0[5]), .ADH6(alu_1_adh0[6]), .ADH7(alu_1_adh0[7]),
    .AI_Debug(alu_1_ai_debug), .BI_Debug(alu_1_bi_debug), .ADD_Debug(alu_1_add_debug),
    .AC_Debug(alu_1_ac_debug), .ADH_In(const_gen_1_adh_out), .SB_Dirty(Dirty[0]), .DB_Dirty(Dirty[1]),
    .ADH_Dirty(Dirty[2]));
  Register #(.trigger("high")) AI (.D(alu_1_ai_debug), .en(1'b1), .clk(1'b1));  // open: Q, clr
  DFF_Level dff_level_3 (.EN(PHI2), .D(nRES), .Q(dff_level_3_q));  // open: NOT_Q
  D_Latch prdy_latch2 (.EN(PHI1), .D(prdy_latch1_not_q), .NOT_Q(prdy_latch2_not_q));  // open: Q
  Register #(.trigger("high")) ADD (.D(alu_1_add_debug), .en(1'b1), .clk(1'b1));  // open: Q, clr
  Register #(.trigger("high")) BI (.D(alu_1_bi_debug), .en(1'b1), .clk(1'b1));  // open: Q, clr
  Register #(.trigger("high")) AC (.D(alu_1_ac_debug), .en(1'b1), .clk(1'b1));  // open: Q, clr
  D_Latch resp_latch (.EN(PHI1), .D(dff_level_3_q), .NOT_Q(resp_latch_not_q));  // open: Q
  BUS_MUX_HACK bus_mux_hack_1 (
    .Y_SB(random_logic_1_y_sb[0]), .X_SB(random_logic_1_y_sb[2]), .S_SB(random_logic_1_y_sb[7]),
    .AC_DB(random_logic_1_sb_adh[2]), .AC_SB(random_logic_1_sb_adh[3]), .ADD_SB06(random_logic_1_ndb_add[5]),
    .ADD_SB7(random_logic_1_ndb_add[6]), .PCL_DB(random_logic_1_adh_pch[7]),
    .PCH_DB(random_logic_1_adh_pch[3]), .PCH_ADH(random_logic_1_adh_pch[2]),
    .DL_ADH(random_logic_1_dl_adl[2]), .DL_DB(random_logic_1_dl_adl[1]), .SB_Dirty(Dirty[0]),
    .DB_Dirty(Dirty[1]), .ADH_Dirty(Dirty[2]), .SBDB_Clutch(bus_mux_hack_1_sbdb_clutch));
  PC pc_1 (
    .PHI2(PHI2), .ADH_PCH(random_logic_1_adh_pch[0]), .PCH_PCH(random_logic_1_adh_pch[1]),
    .PCH_ADH(random_logic_1_adh_pch[2]), .PCH_DB(random_logic_1_adh_pch[3]),
    .ADL_PCL(random_logic_1_adh_pch[4]), .PCL_PCL(random_logic_1_adh_pch[5]),
    .PCL_ADL(random_logic_1_adh_pch[6]), .PCL_DB(random_logic_1_adh_pch[7]),
    ._1_PC(random_logic_1_adh_pch[8]), .ADL0(const_gen_1_adl_out[0]), .ADL1(const_gen_1_adl_out[1]),
    .ADL2(const_gen_1_adl_out[2]), .ADL3(const_gen_1_adl_out[3]), .ADL4(const_gen_1_adl_out[4]),
    .ADL5(const_gen_1_adl_out[5]), .ADL6(const_gen_1_adl_out[6]), .ADL7(const_gen_1_adl_out[7]),
    .ADH0(const_gen_1_adh_out[0]), .ADH1(const_gen_1_adh_out[1]), .ADH2(const_gen_1_adh_out[2]),
    .ADH3(const_gen_1_adh_out[3]), .ADH4(const_gen_1_adh_out[4]), .ADH5(const_gen_1_adh_out[5]),
    .ADH6(const_gen_1_adh_out[6]), .ADH7(const_gen_1_adh_out[7]), .DB0(random_logic_1_db0_2[0]),
    .DB1(random_logic_1_db0_2[1]), .DB2(random_logic_1_db0_2[2]), .DB3(random_logic_1_db0_2[3]),
    .DB4(random_logic_1_db0_2[4]), .DB5(random_logic_1_db0_2[5]), .DB6(random_logic_1_db0_2[6]),
    .DB7(random_logic_1_db0_2[7]), .ADL0_2(regs_1_adl0[0]), .ADL1_2(regs_1_adl0[1]), .ADL2_2(regs_1_adl0[2]),
    .ADL3_2(regs_1_adl0[3]), .ADL4_2(regs_1_adl0[4]), .ADL5_2(regs_1_adl0[5]), .ADL6_2(regs_1_adl0[6]),
    .ADL7_2(regs_1_adl0[7]), .ADH0_2(alu_1_adh0[0]), .ADH1_2(alu_1_adh0[1]), .ADH2_2(alu_1_adh0[2]),
    .ADH3_2(alu_1_adh0[3]), .ADH4_2(alu_1_adh0[4]), .ADH5_2(alu_1_adh0[5]), .ADH6_2(alu_1_adh0[6]),
    .ADH7_2(alu_1_adh0[7]), .PC_Debug(pc_1_pc_debug), .PCS_Debug(pc_1_pcs_debug));
  LED led_1 (.in(bus_mux_hack_1_sbdb_clutch));
  Register #(.width(16), .trigger("high")) PCS (.D(pc_1_pcs_debug), .en(1'b1), .clk(1'b1));  // open: Q, clr
  Register #(.width(16), .trigger("high")) PC_2 (.D(pc_1_pc_debug), .en(1'b1), .clk(1'b1));  // open: Q, clr
  CLOCKGEN clockgen_1 (.PHI0(PHI0), .PHI2(PHI2), .PHI1(PHI1));
  not not_3 (not_3_out, IR_ir5);
  DL dl_1 (
    .PHI1(PHI1), .PHI2(PHI2), .DL_ADL(random_logic_1_dl_adl[0]), .DL_ADH(random_logic_1_dl_adl[2]),
    .DL_DB(random_logic_1_dl_adl[1]), .DB0(precharge_1_db_out[0]), .DB1(precharge_1_db_out[1]),
    .DB2(precharge_1_db_out[2]), .DB3(precharge_1_db_out[3]), .DB4(precharge_1_db_out[4]),
    .DB5(precharge_1_db_out[5]), .DB6(precharge_1_db_out[6]), .DB0_2(random_logic_1_db0_2[0]),
    .DB1_2(random_logic_1_db0_2[1]), .DB2_2(random_logic_1_db0_2[2]), .DB3_2(random_logic_1_db0_2[3]),
    .DB4_2(random_logic_1_db0_2[4]), .DB5_2(random_logic_1_db0_2[5]), .DB6_2(random_logic_1_db0_2[6]),
    .DB7_2(random_logic_1_db0_2[7]), .ADL0(regs_1_adl0[0]), .ADL1(regs_1_adl0[1]), .ADL2(regs_1_adl0[2]),
    .ADL3(regs_1_adl0[3]), .ADL4(regs_1_adl0[4]), .ADL5(regs_1_adl0[5]), .ADL6(regs_1_adl0[6]),
    .ADL7(regs_1_adl0[7]), .ADH0(alu_1_adh0[0]), .ADH1(alu_1_adh0[1]), .ADH2(alu_1_adh0[2]),
    .ADH3(alu_1_adh0[3]), .ADH4(alu_1_adh0[4]), .ADH5(alu_1_adh0[5]), .ADH6(alu_1_adh0[6]),
    .ADH7(alu_1_adh0[7]), .DB7(precharge_1_db_out[7]), .D0(D0), .D1(D1), .D2(D2), .D3(D3), .D4(D4), .D5(D5),
    .D6(D6), .D7(D7), .D0_2(D0_2), .D1_2(D1_2), .D2_2(D2_2), .D3_2(D3_2), .D4_2(D4_2), .D5_2(D5_2),
    .D6_2(D6_2), .D7_2(D7_2), .DL_Debug(dl_1_dl_debug), .DOR_Debug(dl_1_dor_debug), .WR(random_logic_1_wr));
  D_Latch RWLatch (.EN(PHI1), .D(random_logic_1_wr), .NOT_Q(R_W));  // open: Q
  IR IR (
    .FETCH(random_logic_1_fetch), .PHI1(PHI1), .nin0(PREDECODE_npd0), .nin1(PREDECODE_npd1),
    .nin2(PREDECODE_npd2), .nin3(PREDECODE_npd3), .nin4(PREDECODE_npd4), .nin5(PREDECODE_npd5),
    .nin6(PREDECODE_npd6), .nin7(PREDECODE_npd7), .IR0(IR_ir0), .IR2(IR_ir2), .IR3(IR_ir3), .IR4(IR_ir4),
    .IR5(IR_ir5), .IR6(IR_ir6), .IR7(IR_ir7), .IR1(IR_ir1));
  Register #(.trigger("high")) DOR (.D(dl_1_dor_debug), .en(1'b1), .clk(1'b1));  // open: Q, clr
  Register #(.trigger("high")) DL_2 (.D(dl_1_dl_debug), .en(1'b1), .clk(1'b1));  // open: Q, clr
  PREDECODE PREDECODE (
    .PHI2(PHI2), ._0_IR(random_logic_1__0_ir), .D0(D0), .D1(D1), .D2(D2), .D3(D3), .D4(D4), .D5(D5), .D6(D6),
    .D7(D7), .nPD0(PREDECODE_npd0), .nPD1(PREDECODE_npd1), .nPD2(PREDECODE_npd2), .nPD3(PREDECODE_npd3),
    .nPD4(PREDECODE_npd4), .nPD5(PREDECODE_npd5), .nPD6(PREDECODE_npd6), .nPD7(PREDECODE_npd7),
    .nIMPLIED(PREDECODE_nimplied), .nTWOCYCLE(PREDECODE_ntwocycle));

  // Notes on the sheet:
  //   PHI2
  //   PHI1
  //   PHI1
  //   PHI2
  //   T1
  //   The pin layout corresponds to the real chip
  //   /NMIP
  //   /IRQP
  //   ADH in/out
  //   ADL in/out
  //   DB in/out
  //   SB in/out
  //   DEBUG
  //   /PRDY
  //   DEBUG
  //   RESP
  //   DEBUG
  //   PHI2
  //   PHI1
  //   DEBUG
  //   WR
  //   PHI1
  //   PHI2
endmodule

module CLOCKGEN (
  input  PHI0,
  output PHI2,
  output PHI1
);

  wire not_1_out;

  not not_1 (not_1_out, PHI0);
  not not_2 (PHI1, PHI0);
  not not_3 (PHI2, not_1_out);
endmodule

module IR (
  input  FETCH,
  input  PHI1,
  input  nin0,
  input  nin1,
  input  nin2,
  input  nin3,
  input  nin4,
  input  nin5,
  input  nin6,
  input  nin7,
  output IR0,
  output IR1,
  output IR2,
  output IR3,
  output IR4,
  output IR5,
  output IR6,
  output IR7
);

  wire and1_out;

  and and1 (and1_out, FETCH, PHI1);
  D_Latch d_latch_1 (.EN(and1_out), .D(nin0), .NOT_Q(IR0));  // open: Q
  D_Latch d_latch_2 (.EN(and1_out), .D(nin1), .NOT_Q(IR1));  // open: Q
  D_Latch d_latch_3 (.EN(and1_out), .D(nin2), .NOT_Q(IR2));  // open: Q
  D_Latch d_latch_4 (.EN(and1_out), .D(nin3), .NOT_Q(IR3));  // open: Q
  D_Latch d_latch_5 (.EN(and1_out), .D(nin4), .NOT_Q(IR4));  // open: Q
  D_Latch d_latch_6 (.EN(and1_out), .D(nin5), .NOT_Q(IR5));  // open: Q
  D_Latch d_latch_7 (.EN(and1_out), .D(nin6), .NOT_Q(IR6));  // open: Q
  D_Latch d_latch_8 (.EN(and1_out), .D(nin7), .NOT_Q(IR7));  // open: Q
endmodule
// DECODER
module DECODER_TRANS (
  input  nT5,
  input  nT4,
  input  nT3,
  input  nT2,
  input  IR0,
  input  IR1,
  input  IR7,
  input  IR4,
  input  IR3,
  input  IR2,
  input  IR6,
  input  IR5,
  input  nT0,
  input  nT1X,
  output _0,
  output _1,
  output _2,
  output _3,
  output _4,
  output _5,
  output _6,
  output _7,
  output _8,
  output _9,
  output _10,
  output _11,
  output _12,
  output _13,
  output _14,
  output _15,
  output _16,
  output _17,
  output _18,
  output _19,
  output _20,
  output _21,
  output _22,
  output _23,
  output _24,
  output _25,
  output _26,
  output _27,
  output _28,
  output _29,
  output _30,
  output _31,
  output _32,
  output _33,
  output _34,
  output _35,
  output _36,
  output _37,
  output _38,
  output _39,
  output _40,
  output _41,
  output _42,
  output _43,
  output _44,
  output _45,
  output _46,
  output _47,
  output _48,
  output _49,
  output _50,
  output _51,
  output _52,
  output _53,
  output _54,
  output _55,
  output _56,
  output _57,
  output _58,
  output _59,
  output _60,
  output _61,
  output _62,
  output _63,
  output _64,
  output _65,
  output _66,
  output _67,
  output _68,
  output _69,
  output _70,
  output _71,
  output _72,
  output _73,
  output _74,
  output _75,
  output _76,
  output _77,
  output _78,
  output _79,
  output _80,
  output _81,
  output _82,
  output _83,
  output _84,
  output _85,
  output _86,
  output _87,
  output _88,
  output _89,
  output _90,
  output _91,
  output _92,
  output _93,
  output _94,
  output _95,
  output _96,
  output _97,
  output _98,
  output _99,
  output _100,
  output _101,
  output _102,
  output _103,
  output _104,
  output _105,
  output _106,
  output _107,
  output _108,
  output _109,
  output _110,
  output _111,
  output _112,
  output _113,
  output _114,
  output _115,
  output _116,
  output _117,
  output _118,
  output _119,
  output _120,
  output _121,
  output _122,
  output _123,
  output _124,
  output _125,
  output _126,
  output _127,
  output _128,
  output _129
);

  wire not_1_out, not_2_out, not_3_out, not_4_out, not_5_out, not_6_out, not_7_out, not_8_out, or_1_out;

  not not_1 (not_1_out, IR1);
  or or_1 (or_1_out, IR0, IR1);
  not not_2 (not_2_out, IR0);
  not not_3 (not_3_out, IR7);
  not not_4 (not_4_out, IR4);
  not not_5 (not_5_out, IR3);
  not not_6 (not_6_out, IR2);
  not not_7 (not_7_out, IR6);
  not not_8 (not_8_out, IR5);
  Pull_Resistor #(.pull(1)) pull_resistor_1 (.node(_0));
  Pull_Resistor #(.pull(1)) pull_resistor_2 (.node(_1));
  Transistor #(.\type ("n")) transistor_1 (.in(1'b0), .out(_1), .gate(nT3));
  Transistor #(.\type ("n")) transistor_2 (.in(1'b0), .out(_0), .gate(or_1_out));
  Transistor #(.\type ("n")) transistor_3 (.in(1'b0), .out(_1), .gate(not_2_out));
  Transistor #(.\type ("n")) transistor_4 (.in(1'b0), .out(_0), .gate(not_3_out));
  Transistor #(.\type ("n")) transistor_5 (.in(1'b0), .out(_1), .gate(not_4_out));
  Transistor #(.\type ("n")) transistor_6 (.in(1'b0), .out(_1), .gate(IR3));
  Transistor #(.\type ("n")) transistor_7 (.in(1'b0), .out(_1), .gate(IR2));
  Transistor #(.\type ("n")) transistor_8 (.in(1'b0), .out(_0), .gate(not_6_out));
  Transistor #(.\type ("n")) transistor_9 (.in(1'b0), .out(_0), .gate(IR6));
  Transistor #(.\type ("n")) transistor_10 (.in(1'b0), .out(_0), .gate(IR5));
  Pull_Resistor #(.pull(1)) pull_resistor_3 (.node(_2));
  Transistor #(.\type ("n")) transistor_11 (.in(1'b0), .out(_2), .gate(nT2));
  Transistor #(.\type ("n")) transistor_12 (.in(1'b0), .out(_2), .gate(not_2_out));
  Transistor #(.\type ("n")) transistor_13 (.in(1'b0), .out(_2), .gate(not_4_out));
  Transistor #(.\type ("n")) transistor_14 (.in(1'b0), .out(_2), .gate(not_5_out));
  Transistor #(.\type ("n")) transistor_15 (.in(1'b0), .out(_2), .gate(IR2));
  Pull_Resistor #(.pull(1)) pull_resistor_4 (.node(_3));
  Transistor #(.\type ("n")) transistor_16 (.in(1'b0), .out(_3), .gate(or_1_out));
  Transistor #(.\type ("n")) transistor_17 (.in(1'b0), .out(_3), .gate(not_3_out));
  Transistor #(.\type ("n")) transistor_18 (.in(1'b0), .out(_3), .gate(IR4));
  Transistor #(.\type ("n")) transistor_19 (.in(1'b0), .out(_3), .gate(not_5_out));
  Transistor #(.\type ("n")) transistor_20 (.in(1'b0), .out(_3), .gate(IR2));
  Transistor #(.\type ("n")) transistor_21 (.in(1'b0), .out(_3), .gate(IR5));
  Transistor #(.\type ("n")) transistor_22 (.in(1'b0), .out(_3), .gate(nT0));
  Pull_Resistor #(.pull(1)) pull_resistor_5 (.node(_5));
  Pull_Resistor #(.pull(1)) pull_resistor_6 (.node(_4));
  Transistor #(.\type ("n")) transistor_23 (.in(1'b0), .out(_4), .gate(or_1_out));
  Transistor #(.\type ("n")) transistor_24 (.in(1'b0), .out(_5), .gate(or_1_out));
  Transistor #(.\type ("n")) transistor_25 (.in(1'b0), .out(_4), .gate(not_3_out));
  Transistor #(.\type ("n")) transistor_26 (.in(1'b0), .out(_5), .gate(not_3_out));
  Transistor #(.\type ("n")) transistor_27 (.in(1'b0), .out(_5), .gate(IR4));
  Transistor #(.\type ("n")) transistor_28 (.in(1'b0), .out(_4), .gate(not_4_out));
  Transistor #(.\type ("n")) transistor_29 (.in(1'b0), .out(_4), .gate(not_5_out));
  Transistor #(.\type ("n")) transistor_30 (.in(1'b0), .out(_4), .gate(IR2));
  Transistor #(.\type ("n")) transistor_31 (.in(1'b0), .out(_4), .gate(IR6));
  Transistor #(.\type ("n")) transistor_32 (.in(1'b0), .out(_5), .gate(not_7_out));
  Transistor #(.\type ("n")) transistor_33 (.in(1'b0), .out(_4), .gate(IR5));
  Transistor #(.\type ("n")) transistor_34 (.in(1'b0), .out(_5), .gate(IR5));
  Transistor #(.\type ("n")) transistor_35 (.in(1'b0), .out(_5), .gate(nT0));
  Transistor #(.\type ("n")) transistor_36 (.in(1'b0), .out(_4), .gate(nT0));
  Pull_Resistor #(.pull(1)) pull_resistor_7 (.node(_6));
  Transistor #(.\type ("n")) transistor_37 (.in(1'b0), .out(_6), .gate(nT2));
  Transistor #(.\type ("n")) transistor_38 (.in(1'b0), .out(_6), .gate(not_4_out));
  Transistor #(.\type ("n")) transistor_39 (.in(1'b0), .out(_6), .gate(not_6_out));
  Pull_Resistor #(.pull(1)) pull_resistor_8 (.node(_7));
  Transistor #(.\type ("n")) transistor_40 (.in(1'b0), .out(_7), .gate(not_1_out));
  Transistor #(.\type ("n")) transistor_41 (.in(1'b0), .out(_7), .gate(not_3_out));
  Transistor #(.\type ("n")) transistor_42 (.in(1'b0), .out(_7), .gate(IR6));
  Pull_Resistor #(.pull(1)) pull_resistor_9 (.node(_8));
  Pull_Resistor #(.pull(1)) pull_resistor_10 (.node(_9));
  Transistor #(.\type ("n")) transistor_43 (.in(1'b0), .out(_8), .gate(nT2));
  Transistor #(.\type ("n")) transistor_44 (.in(1'b0), .out(_9), .gate(not_1_out));
  Transistor #(.\type ("n")) transistor_45 (.in(1'b0), .out(_8), .gate(not_2_out));
  Transistor #(.\type ("n")) transistor_46 (.in(1'b0), .out(_9), .gate(not_3_out));
  Transistor #(.\type ("n")) transistor_47 (.in(1'b0), .out(_8), .gate(IR4));
  Transistor #(.\type ("n")) transistor_48 (.in(1'b0), .out(_9), .gate(IR4));
  Transistor #(.\type ("n")) transistor_49 (.in(1'b0), .out(_8), .gate(IR3));
  Transistor #(.\type ("n")) transistor_50 (.in(1'b0), .out(_9), .gate(not_5_out));
  Transistor #(.\type ("n")) transistor_51 (.in(1'b0), .out(_9), .gate(IR2));
  Transistor #(.\type ("n")) transistor_52 (.in(1'b0), .out(_8), .gate(IR2));
  Transistor #(.\type ("n")) transistor_53 (.in(1'b0), .out(_9), .gate(IR6));
  Transistor #(.\type ("n")) transistor_54 (.in(1'b0), .out(_9), .gate(IR5));
  Transistor #(.\type ("n")) transistor_55 (.in(1'b0), .out(_9), .gate(nT0));
  Pull_Resistor #(.pull(1)) pull_resistor_11 (.node(_10));
  Transistor #(.\type ("n")) transistor_56 (.in(1'b0), .out(_10), .gate(not_1_out));
  Transistor #(.\type ("n")) transistor_57 (.in(1'b0), .out(_10), .gate(not_3_out));
  Transistor #(.\type ("n")) transistor_58 (.in(1'b0), .out(_10), .gate(IR4));
  Transistor #(.\type ("n")) transistor_59 (.in(1'b0), .out(_10), .gate(not_5_out));
  Transistor #(.\type ("n")) transistor_60 (.in(1'b0), .out(_10), .gate(IR2));
  Transistor #(.\type ("n")) transistor_61 (.in(1'b0), .out(_10), .gate(not_7_out));
  Transistor #(.\type ("n")) transistor_62 (.in(1'b0), .out(_10), .gate(IR5));
  Transistor #(.\type ("n")) transistor_63 (.in(1'b0), .out(_10), .gate(nT0));
  Pull_Resistor #(.pull(1)) pull_resistor_12 (.node(_11));
  Transistor #(.\type ("n")) transistor_64 (.in(1'b0), .out(_11), .gate(or_1_out));
  Transistor #(.\type ("n")) transistor_65 (.in(1'b0), .out(_11), .gate(not_3_out));
  Transistor #(.\type ("n")) transistor_66 (.in(1'b0), .out(_11), .gate(IR4));
  Transistor #(.\type ("n")) transistor_67 (.in(1'b0), .out(_11), .gate(not_7_out));
  Transistor #(.\type ("n")) transistor_68 (.in(1'b0), .out(_11), .gate(not_8_out));
  Transistor #(.\type ("n")) transistor_69 (.in(1'b0), .out(_11), .gate(nT0));
  Pull_Resistor #(.pull(1)) pull_resistor_13 (.node(_12));
  Pull_Resistor #(.pull(1)) pull_resistor_14 (.node(_13));
  Transistor #(.\type ("n")) transistor_70 (.in(1'b0), .out(_13), .gate(not_1_out));
  Transistor #(.\type ("n")) transistor_71 (.in(1'b0), .out(_12), .gate(not_1_out));
  Transistor #(.\type ("n")) transistor_72 (.in(1'b0), .out(_13), .gate(not_3_out));
  Transistor #(.\type ("n")) transistor_73 (.in(1'b0), .out(_12), .gate(not_3_out));
  Transistor #(.\type ("n")) transistor_74 (.in(1'b0), .out(_13), .gate(not_4_out));
  Transistor #(.\type ("n")) transistor_75 (.in(1'b0), .out(_13), .gate(not_5_out));
  Transistor #(.\type ("n")) transistor_76 (.in(1'b0), .out(_13), .gate(IR2));
  Transistor #(.\type ("n")) transistor_77 (.in(1'b0), .out(_13), .gate(IR6));
  Transistor #(.\type ("n")) transistor_78 (.in(1'b0), .out(_12), .gate(IR6));
  Transistor #(.\type ("n")) transistor_79 (.in(1'b0), .out(_13), .gate(IR5));
  Transistor #(.\type ("n")) transistor_80 (.in(1'b0), .out(_12), .gate(IR5));
  Transistor #(.\type ("n")) transistor_81 (.in(1'b0), .out(_13), .gate(nT0));
  Pull_Resistor #(.pull(1)) pull_resistor_15 (.node(_14));
  Transistor #(.\type ("n")) transistor_82 (.in(1'b0), .out(_14), .gate(not_1_out));
  Transistor #(.\type ("n")) transistor_83 (.in(1'b0), .out(_14), .gate(not_3_out));
  Transistor #(.\type ("n")) transistor_84 (.in(1'b0), .out(_14), .gate(IR6));
  Transistor #(.\type ("n")) transistor_85 (.in(1'b0), .out(_14), .gate(not_8_out));
  Transistor #(.\type ("n")) transistor_86 (.in(1'b0), .out(_14), .gate(nT0));
  Pull_Resistor #(.pull(1)) pull_resistor_16 (.node(_15));
  Transistor #(.\type ("n")) transistor_87 (.in(1'b0), .out(_15), .gate(not_1_out));
  Transistor #(.\type ("n")) transistor_88 (.in(1'b0), .out(_15), .gate(not_3_out));
  Transistor #(.\type ("n")) transistor_89 (.in(1'b0), .out(_15), .gate(IR4));
  Transistor #(.\type ("n")) transistor_90 (.in(1'b0), .out(_15), .gate(not_5_out));
  Transistor #(.\type ("n")) transistor_91 (.in(1'b0), .out(_15), .gate(IR2));
  Transistor #(.\type ("n")) transistor_92 (.in(1'b0), .out(_15), .gate(not_7_out));
  Transistor #(.\type ("n")) transistor_93 (.in(1'b0), .out(_15), .gate(IR5));
  Transistor #(.\type ("n")) transistor_94 (.in(1'b0), .out(_15), .gate(nT1X));
  Pull_Resistor #(.pull(1)) pull_resistor_17 (.node(_17));
  Pull_Resistor #(.pull(1)) pull_resistor_18 (.node(_16));
  Transistor #(.\type ("n")) transistor_95 (.in(1'b0), .out(_17), .gate(not_1_out));
  Transistor #(.\type ("n")) transistor_96 (.in(1'b0), .out(_16), .gate(or_1_out));
  Transistor #(.\type ("n")) transistor_97 (.in(1'b0), .out(_17), .gate(not_3_out));
  Transistor #(.\type ("n")) transistor_98 (.in(1'b0), .out(_16), .gate(not_3_out));
  Transistor #(.\type ("n")) transistor_99 (.in(1'b0), .out(_16), .gate(IR4));
  Transistor #(.\type ("n")) transistor_100 (.in(1'b0), .out(_17), .gate(not_4_out));
  Transistor #(.\type ("n")) transistor_101 (.in(1'b0), .out(_16), .gate(not_5_out));
  Transistor #(.\type ("n")) transistor_102 (.in(1'b0), .out(_17), .gate(not_5_out));
  Transistor #(.\type ("n")) transistor_103 (.in(1'b0), .out(_17), .gate(IR2));
  Transistor #(.\type ("n")) transistor_104 (.in(1'b0), .out(_16), .gate(IR2));
  Transistor #(.\type ("n")) transistor_105 (.in(1'b0), .out(_17), .gate(IR6));
  Transistor #(.\type ("n")) transistor_106 (.in(1'b0), .out(_16), .gate(not_7_out));
  Transistor #(.\type ("n")) transistor_107 (.in(1'b0), .out(_16), .gate(not_8_out));
  Transistor #(.\type ("n")) transistor_108 (.in(1'b0), .out(_17), .gate(not_8_out));
  Transistor #(.\type ("n")) transistor_109 (.in(1'b0), .out(_17), .gate(nT0));
  Transistor #(.\type ("n")) transistor_110 (.in(1'b0), .out(_16), .gate(nT1X));
  Pull_Resistor #(.pull(1)) pull_resistor_19 (.node(_18));
  Transistor #(.\type ("n")) transistor_111 (.in(1'b0), .out(_18), .gate(or_1_out));
  Transistor #(.\type ("n")) transistor_112 (.in(1'b0), .out(_18), .gate(not_3_out));
  Transistor #(.\type ("n")) transistor_113 (.in(1'b0), .out(_18), .gate(IR4));
  Transistor #(.\type ("n")) transistor_114 (.in(1'b0), .out(_18), .gate(not_5_out));
  Transistor #(.\type ("n")) transistor_115 (.in(1'b0), .out(_18), .gate(IR2));
  Transistor #(.\type ("n")) transistor_116 (.in(1'b0), .out(_18), .gate(IR5));
  Transistor #(.\type ("n")) transistor_117 (.in(1'b0), .out(_18), .gate(nT1X));
  Pull_Resistor #(.pull(1)) pull_resistor_20 (.node(_19));
  Transistor #(.\type ("n")) transistor_118 (.in(1'b0), .out(_19), .gate(or_1_out));
  Transistor #(.\type ("n")) transistor_119 (.in(1'b0), .out(_19), .gate(not_3_out));
  Transistor #(.\type ("n")) transistor_120 (.in(1'b0), .out(_19), .gate(not_6_out));
  Transistor #(.\type ("n")) transistor_121 (.in(1'b0), .out(_19), .gate(IR6));
  Transistor #(.\type ("n")) transistor_122 (.in(1'b0), .out(_19), .gate(not_8_out));
  Transistor #(.\type ("n")) transistor_123 (.in(1'b0), .out(_19), .gate(nT0));
  Pull_Resistor #(.pull(1)) pull_resistor_21 (.node(_20));
  Transistor #(.\type ("n")) transistor_124 (.in(1'b0), .out(_20), .gate(or_1_out));
  Transistor #(.\type ("n")) transistor_125 (.in(1'b0), .out(_20), .gate(not_3_out));
  Transistor #(.\type ("n")) transistor_126 (.in(1'b0), .out(_20), .gate(IR4));
  Transistor #(.\type ("n")) transistor_127 (.in(1'b0), .out(_20), .gate(IR6));
  Transistor #(.\type ("n")) transistor_128 (.in(1'b0), .out(_20), .gate(not_8_out));
  Transistor #(.\type ("n")) transistor_129 (.in(1'b0), .out(_20), .gate(nT0));
  Pull_Resistor #(.pull(1)) pull_resistor_22 (.node(_21));
  Transistor #(.\type ("n")) transistor_130 (.in(1'b0), .out(_21), .gate(or_1_out));
  Transistor #(.\type ("n")) transistor_131 (.in(1'b0), .out(_21), .gate(IR7));
  Transistor #(.\type ("n")) transistor_132 (.in(1'b0), .out(_21), .gate(IR4));
  Transistor #(.\type ("n")) transistor_133 (.in(1'b0), .out(_21), .gate(IR3));
  Transistor #(.\type ("n")) transistor_134 (.in(1'b0), .out(_21), .gate(IR2));
  Transistor #(.\type ("n")) transistor_135 (.in(1'b0), .out(_21), .gate(IR6));
  Transistor #(.\type ("n")) transistor_136 (.in(1'b0), .out(_21), .gate(not_8_out));
  Transistor #(.\type ("n")) transistor_137 (.in(1'b0), .out(_21), .gate(nT0));
  Pull_Resistor #(.pull(1)) pull_resistor_23 (.node(_22));
  Transistor #(.\type ("n")) transistor_138 (.in(1'b0), .out(_22), .gate(nT5));
  Transistor #(.\type ("n")) transistor_139 (.in(1'b0), .out(_22), .gate(or_1_out));
  Transistor #(.\type ("n")) transistor_140 (.in(1'b0), .out(_22), .gate(IR7));
  Transistor #(.\type ("n")) transistor_141 (.in(1'b0), .out(_22), .gate(IR4));
  Transistor #(.\type ("n")) transistor_142 (.in(1'b0), .out(_22), .gate(IR3));
  Transistor #(.\type ("n")) transistor_143 (.in(1'b0), .out(_22), .gate(IR2));
  Transistor #(.\type ("n")) transistor_144 (.in(1'b0), .out(_22), .gate(IR6));
  Transistor #(.\type ("n")) transistor_145 (.in(1'b0), .out(_22), .gate(IR5));
  Pull_Resistor #(.pull(1)) pull_resistor_24 (.node(_23));
  Transistor #(.\type ("n")) transistor_146 (.in(1'b0), .out(_23), .gate(or_1_out));
  Transistor #(.\type ("n")) transistor_147 (.in(1'b0), .out(_23), .gate(IR7));
  Transistor #(.\type ("n")) transistor_148 (.in(1'b0), .out(_23), .gate(IR4));
  Transistor #(.\type ("n")) transistor_149 (.in(1'b0), .out(_23), .gate(not_5_out));
  Transistor #(.\type ("n")) transistor_150 (.in(1'b0), .out(_23), .gate(IR2));
  Transistor #(.\type ("n")) transistor_151 (.in(1'b0), .out(_23), .gate(IR5));
  Transistor #(.\type ("n")) transistor_152 (.in(1'b0), .out(_23), .gate(nT0));
  Pull_Resistor #(.pull(1)) pull_resistor_25 (.node(_25));
  Pull_Resistor #(.pull(1)) pull_resistor_26 (.node(_24));
  Transistor #(.\type ("n")) transistor_153 (.in(1'b0), .out(_24), .gate(nT4));
  Transistor #(.\type ("n")) transistor_154 (.in(1'b0), .out(_25), .gate(nT3));
  Transistor #(.\type ("n")) transistor_155 (.in(1'b0), .out(_25), .gate(or_1_out));
  Transistor #(.\type ("n")) transistor_156 (.in(1'b0), .out(_24), .gate(or_1_out));
  Transistor #(.\type ("n")) transistor_157 (.in(1'b0), .out(_25), .gate(IR7));
  Transistor #(.\type ("n")) transistor_158 (.in(1'b0), .out(_24), .gate(IR7));
  Transistor #(.\type ("n")) transistor_159 (.in(1'b0), .out(_25), .gate(IR4));
  Transistor #(.\type ("n")) transistor_160 (.in(1'b0), .out(_24), .gate(IR4));
  Transistor #(.\type ("n")) transistor_161 (.in(1'b0), .out(_24), .gate(IR3));
  Transistor #(.\type ("n")) transistor_162 (.in(1'b0), .out(_25), .gate(not_5_out));
  Transistor #(.\type ("n")) transistor_163 (.in(1'b0), .out(_24), .gate(IR2));
  Transistor #(.\type ("n")) transistor_164 (.in(1'b0), .out(_25), .gate(IR2));
  Transistor #(.\type ("n")) transistor_165 (.in(1'b0), .out(_24), .gate(not_7_out));
  Transistor #(.\type ("n")) transistor_166 (.in(1'b0), .out(_25), .gate(not_8_out));
  Transistor #(.\type ("n")) transistor_167 (.in(1'b0), .out(_24), .gate(not_8_out));
  Pull_Resistor #(.pull(1)) pull_resistor_27 (.node(_26));
  Transistor #(.\type ("n")) transistor_168 (.in(1'b0), .out(_26), .gate(nT5));
  Transistor #(.\type ("n")) transistor_169 (.in(1'b0), .out(_26), .gate(or_1_out));
  Transistor #(.\type ("n")) transistor_170 (.in(1'b0), .out(_26), .gate(IR7));
  Transistor #(.\type ("n")) transistor_171 (.in(1'b0), .out(_26), .gate(IR4));
  Transistor #(.\type ("n")) transistor_172 (.in(1'b0), .out(_26), .gate(IR3));
  Transistor #(.\type ("n")) transistor_173 (.in(1'b0), .out(_26), .gate(IR2));
  Transistor #(.\type ("n")) transistor_174 (.in(1'b0), .out(_26), .gate(not_7_out));
  Transistor #(.\type ("n")) transistor_175 (.in(1'b0), .out(_26), .gate(IR5));
  Pull_Resistor #(.pull(1)) pull_resistor_28 (.node(_27));
  Transistor #(.\type ("n")) transistor_176 (.in(1'b0), .out(_27), .gate(not_1_out));
  Transistor #(.\type ("n")) transistor_177 (.in(1'b0), .out(_27), .gate(IR7));
  Transistor #(.\type ("n")) transistor_178 (.in(1'b0), .out(_27), .gate(not_7_out));
  Transistor #(.\type ("n")) transistor_179 (.in(1'b0), .out(_27), .gate(not_8_out));
  Pull_Resistor #(.pull(1)) pull_resistor_29 (.node(_28));
  Pull_Resistor #(.pull(1)) pull_resistor_30 (.node(_29));
  Transistor #(.\type ("n")) transistor_180 (.in(1'b0), .out(_28), .gate(nT2));
  Transistor #(.\type ("n")) transistor_181 (.in(1'b0), .out(_29), .gate(not_2_out));
  Transistor #(.\type ("n")) transistor_182 (.in(1'b0), .out(_29), .gate(IR7));
  Transistor #(.\type ("n")) transistor_183 (.in(1'b0), .out(_29), .gate(not_7_out));
  Transistor #(.\type ("n")) transistor_184 (.in(1'b0), .out(_29), .gate(IR5));
  Transistor #(.\type ("n")) transistor_185 (.in(1'b0), .out(_29), .gate(nT0));
  Pull_Resistor #(.pull(1)) pull_resistor_31 (.node(_30));
  Transistor #(.\type ("n")) transistor_186 (.in(1'b0), .out(_30), .gate(or_1_out));
  Transistor #(.\type ("n")) transistor_187 (.in(1'b0), .out(_30), .gate(IR7));
  Transistor #(.\type ("n")) transistor_188 (.in(1'b0), .out(_30), .gate(IR4));
  Transistor #(.\type ("n")) transistor_189 (.in(1'b0), .out(_30), .gate(not_5_out));
  Transistor #(.\type ("n")) transistor_190 (.in(1'b0), .out(_30), .gate(not_6_out));
  Transistor #(.\type ("n")) transistor_191 (.in(1'b0), .out(_30), .gate(not_7_out));
  Pull_Resistor #(.pull(1)) pull_resistor_32 (.node(_31));
  Transistor #(.\type ("n")) transistor_192 (.in(1'b0), .out(_31), .gate(nT2));
  Transistor #(.\type ("n")) transistor_193 (.in(1'b0), .out(_31), .gate(IR4));
  Transistor #(.\type ("n")) transistor_194 (.in(1'b0), .out(_31), .gate(not_5_out));
  Transistor #(.\type ("n")) transistor_195 (.in(1'b0), .out(_31), .gate(not_6_out));
  Pull_Resistor #(.pull(1)) pull_resistor_33 (.node(_33));
  Pull_Resistor #(.pull(1)) pull_resistor_34 (.node(_32));
  Transistor #(.\type ("n")) transistor_196 (.in(1'b0), .out(_33), .gate(nT2));
  Transistor #(.\type ("n")) transistor_197 (.in(1'b0), .out(_32), .gate(not_2_out));
  Transistor #(.\type ("n")) transistor_198 (.in(1'b0), .out(_32), .gate(IR7));
  Transistor #(.\type ("n")) transistor_199 (.in(1'b0), .out(_33), .gate(IR3));
  Transistor #(.\type ("n")) transistor_200 (.in(1'b0), .out(_32), .gate(IR6));
  Transistor #(.\type ("n")) transistor_201 (.in(1'b0), .out(_32), .gate(IR5));
  Transistor #(.\type ("n")) transistor_202 (.in(1'b0), .out(_32), .gate(nT0));
  Pull_Resistor #(.pull(1)) pull_resistor_35 (.node(_34));
  Transistor #(.\type ("n")) transistor_203 (.in(1'b0), .out(_34), .gate(nT0));
  Pull_Resistor #(.pull(1)) pull_resistor_36 (.node(_35));
  Transistor #(.\type ("n")) transistor_204 (.in(1'b0), .out(_35), .gate(nT2));
  Transistor #(.\type ("n")) transistor_205 (.in(1'b0), .out(_35), .gate(or_1_out));
  Transistor #(.\type ("n")) transistor_206 (.in(1'b0), .out(_35), .gate(IR7));
  Transistor #(.\type ("n")) transistor_207 (.in(1'b0), .out(_35), .gate(IR4));
  Transistor #(.\type ("n")) transistor_208 (.in(1'b0), .out(_35), .gate(IR2));
  Pull_Resistor #(.pull(1)) pull_resistor_37 (.node(_36));
  Transistor #(.\type ("n")) transistor_209 (.in(1'b0), .out(_36), .gate(nT3));
  Transistor #(.\type ("n")) transistor_210 (.in(1'b0), .out(_36), .gate(or_1_out));
  Transistor #(.\type ("n")) transistor_211 (.in(1'b0), .out(_36), .gate(IR7));
  Transistor #(.\type ("n")) transistor_212 (.in(1'b0), .out(_36), .gate(IR4));
  Pull_Resistor #(.pull(1)) pull_resistor_38 (.node(_37));
  Transistor #(.\type ("n")) transistor_213 (.in(1'b0), .out(_37), .gate(nT4));
  Transistor #(.\type ("n")) transistor_214 (.in(1'b0), .out(_37), .gate(or_1_out));
  Transistor #(.\type ("n")) transistor_215 (.in(1'b0), .out(_37), .gate(IR7));
  Transistor #(.\type ("n")) transistor_216 (.in(1'b0), .out(_37), .gate(IR4));
  Transistor #(.\type ("n")) transistor_217 (.in(1'b0), .out(_37), .gate(IR3));
  Transistor #(.\type ("n")) transistor_218 (.in(1'b0), .out(_37), .gate(IR2));
  Transistor #(.\type ("n")) transistor_219 (.in(1'b0), .out(_37), .gate(IR6));
  Pull_Resistor #(.pull(1)) pull_resistor_39 (.node(_38));
  Transistor #(.\type ("n")) transistor_220 (.in(1'b0), .out(_38), .gate(nT4));
  Transistor #(.\type ("n")) transistor_221 (.in(1'b0), .out(_38), .gate(or_1_out));
  Transistor #(.\type ("n")) transistor_222 (.in(1'b0), .out(_38), .gate(IR7));
  Transistor #(.\type ("n")) transistor_223 (.in(1'b0), .out(_38), .gate(IR4));
  Transistor #(.\type ("n")) transistor_224 (.in(1'b0), .out(_38), .gate(IR3));
  Transistor #(.\type ("n")) transistor_225 (.in(1'b0), .out(_38), .gate(IR2));
  Transistor #(.\type ("n")) transistor_226 (.in(1'b0), .out(_38), .gate(not_7_out));
  Transistor #(.\type ("n")) transistor_227 (.in(1'b0), .out(_38), .gate(IR5));
  Pull_Resistor #(.pull(1)) pull_resistor_40 (.node(_40));
  Pull_Resistor #(.pull(1)) pull_resistor_41 (.node(_39));
  Transistor #(.\type ("n")) transistor_228 (.in(1'b0), .out(_40), .gate(nT4));
  Transistor #(.\type ("n")) transistor_229 (.in(1'b0), .out(_39), .gate(nT3));
  Transistor #(.\type ("n")) transistor_230 (.in(1'b0), .out(_40), .gate(not_2_out));
  Transistor #(.\type ("n")) transistor_231 (.in(1'b0), .out(_39), .gate(not_2_out));
  Transistor #(.\type ("n")) transistor_232 (.in(1'b0), .out(_39), .gate(IR4));
  Transistor #(.\type ("n")) transistor_233 (.in(1'b0), .out(_40), .gate(not_4_out));
  Transistor #(.\type ("n")) transistor_234 (.in(1'b0), .out(_40), .gate(IR3));
  Transistor #(.\type ("n")) transistor_235 (.in(1'b0), .out(_39), .gate(IR3));
  Transistor #(.\type ("n")) transistor_236 (.in(1'b0), .out(_40), .gate(IR2));
  Transistor #(.\type ("n")) transistor_237 (.in(1'b0), .out(_39), .gate(IR2));
  Pull_Resistor #(.pull(1)) pull_resistor_42 (.node(_41));
  Transistor #(.\type ("n")) transistor_238 (.in(1'b0), .out(_41), .gate(nT2));
  Transistor #(.\type ("n")) transistor_239 (.in(1'b0), .out(_41), .gate(not_2_out));
  Transistor #(.\type ("n")) transistor_240 (.in(1'b0), .out(_41), .gate(not_4_out));
  Transistor #(.\type ("n")) transistor_241 (.in(1'b0), .out(_41), .gate(IR3));
  Transistor #(.\type ("n")) transistor_242 (.in(1'b0), .out(_41), .gate(IR2));
  Pull_Resistor #(.pull(1)) pull_resistor_43 (.node(_42));
  Transistor #(.\type ("n")) transistor_243 (.in(1'b0), .out(_42), .gate(nT3));
  Transistor #(.\type ("n")) transistor_244 (.in(1'b0), .out(_42), .gate(not_4_out));
  Transistor #(.\type ("n")) transistor_245 (.in(1'b0), .out(_42), .gate(not_5_out));
  Pull_Resistor #(.pull(1)) pull_resistor_44 (.node(_43));
  Pull_Resistor #(.pull(1)) pull_resistor_45 (.node(_44));
  Transistor #(.\type ("n")) transistor_246 (.in(1'b0), .out(_44), .gate(not_1_out));
  Transistor #(.\type ("n")) transistor_247 (.in(1'b0), .out(_43), .gate(or_1_out));
  Transistor #(.\type ("n")) transistor_248 (.in(1'b0), .out(_43), .gate(IR7));
  Transistor #(.\type ("n")) transistor_249 (.in(1'b0), .out(_44), .gate(not_3_out));
  Transistor #(.\type ("n")) transistor_250 (.in(1'b0), .out(_43), .gate(IR4));
  Transistor #(.\type ("n")) transistor_251 (.in(1'b0), .out(_43), .gate(not_5_out));
  Transistor #(.\type ("n")) transistor_252 (.in(1'b0), .out(_43), .gate(IR2));
  Transistor #(.\type ("n")) transistor_253 (.in(1'b0), .out(_44), .gate(not_7_out));
  Transistor #(.\type ("n")) transistor_254 (.in(1'b0), .out(_44), .gate(not_8_out));
  Transistor #(.\type ("n")) transistor_255 (.in(1'b0), .out(_43), .gate(not_8_out));
  Pull_Resistor #(.pull(1)) pull_resistor_46 (.node(_45));
  Transistor #(.\type ("n")) transistor_256 (.in(1'b0), .out(_45), .gate(nT4));
  Transistor #(.\type ("n")) transistor_257 (.in(1'b0), .out(_45), .gate(not_2_out));
  Transistor #(.\type ("n")) transistor_258 (.in(1'b0), .out(_45), .gate(IR4));
  Transistor #(.\type ("n")) transistor_259 (.in(1'b0), .out(_45), .gate(IR3));
  Transistor #(.\type ("n")) transistor_260 (.in(1'b0), .out(_45), .gate(IR2));
  Pull_Resistor #(.pull(1)) pull_resistor_47 (.node(_46));
  Transistor #(.\type ("n")) transistor_261 (.in(1'b0), .out(_46), .gate(nT3));
  Transistor #(.\type ("n")) transistor_262 (.in(1'b0), .out(_46), .gate(not_2_out));
  Transistor #(.\type ("n")) transistor_263 (.in(1'b0), .out(_46), .gate(not_4_out));
  Transistor #(.\type ("n")) transistor_264 (.in(1'b0), .out(_46), .gate(IR3));
  Transistor #(.\type ("n")) transistor_265 (.in(1'b0), .out(_46), .gate(IR2));
  Pull_Resistor #(.pull(1)) pull_resistor_48 (.node(_47));
  Pull_Resistor #(.pull(1)) pull_resistor_49 (.node(_48));
  Transistor #(.\type ("n")) transistor_266 (.in(1'b0), .out(_48), .gate(nT2));
  Transistor #(.\type ("n")) transistor_267 (.in(1'b0), .out(_48), .gate(or_1_out));
  Transistor #(.\type ("n")) transistor_268 (.in(1'b0), .out(_47), .gate(or_1_out));
  Transistor #(.\type ("n")) transistor_269 (.in(1'b0), .out(_48), .gate(IR7));
  Transistor #(.\type ("n")) transistor_270 (.in(1'b0), .out(_47), .gate(IR7));
  Transistor #(.\type ("n")) transistor_271 (.in(1'b0), .out(_47), .gate(IR4));
  Transistor #(.\type ("n")) transistor_272 (.in(1'b0), .out(_48), .gate(IR4));
  Transistor #(.\type ("n")) transistor_273 (.in(1'b0), .out(_48), .gate(IR3));
  Transistor #(.\type ("n")) transistor_274 (.in(1'b0), .out(_47), .gate(IR3));
  Transistor #(.\type ("n")) transistor_275 (.in(1'b0), .out(_47), .gate(IR2));
  Transistor #(.\type ("n")) transistor_276 (.in(1'b0), .out(_48), .gate(IR2));
  Transistor #(.\type ("n")) transistor_277 (.in(1'b0), .out(_48), .gate(IR6));
  Transistor #(.\type ("n")) transistor_278 (.in(1'b0), .out(_47), .gate(not_7_out));
  Transistor #(.\type ("n")) transistor_279 (.in(1'b0), .out(_48), .gate(not_8_out));
  Pull_Resistor #(.pull(1)) pull_resistor_50 (.node(_49));
  Transistor #(.\type ("n")) transistor_280 (.in(1'b0), .out(_49), .gate(or_1_out));
  Transistor #(.\type ("n")) transistor_281 (.in(1'b0), .out(_49), .gate(not_3_out));
  Transistor #(.\type ("n")) transistor_282 (.in(1'b0), .out(_49), .gate(IR4));
  Transistor #(.\type ("n")) transistor_283 (.in(1'b0), .out(_49), .gate(not_7_out));
  Transistor #(.\type ("n")) transistor_284 (.in(1'b0), .out(_49), .gate(nT0));
  Pull_Resistor #(.pull(1)) pull_resistor_51 (.node(_50));
  Transistor #(.\type ("n")) transistor_285 (.in(1'b0), .out(_50), .gate(not_2_out));
  Transistor #(.\type ("n")) transistor_286 (.in(1'b0), .out(_50), .gate(not_3_out));
  Transistor #(.\type ("n")) transistor_287 (.in(1'b0), .out(_50), .gate(not_7_out));
  Transistor #(.\type ("n")) transistor_288 (.in(1'b0), .out(_50), .gate(IR5));
  Transistor #(.\type ("n")) transistor_289 (.in(1'b0), .out(_50), .gate(nT0));
  Pull_Resistor #(.pull(1)) pull_resistor_52 (.node(_51));
  Pull_Resistor #(.pull(1)) pull_resistor_53 (.node(_52));
  Transistor #(.\type ("n")) transistor_290 (.in(1'b0), .out(_52), .gate(not_2_out));
  Transistor #(.\type ("n")) transistor_291 (.in(1'b0), .out(_51), .gate(not_2_out));
  Transistor #(.\type ("n")) transistor_292 (.in(1'b0), .out(_51), .gate(not_3_out));
  Transistor #(.\type ("n")) transistor_293 (.in(1'b0), .out(_52), .gate(not_7_out));
  Transistor #(.\type ("n")) transistor_294 (.in(1'b0), .out(_51), .gate(not_7_out));
  Transistor #(.\type ("n")) transistor_295 (.in(1'b0), .out(_51), .gate(not_8_out));
  Transistor #(.\type ("n")) transistor_296 (.in(1'b0), .out(_52), .gate(not_8_out));
  Transistor #(.\type ("n")) transistor_297 (.in(1'b0), .out(_51), .gate(nT0));
  Transistor #(.\type ("n")) transistor_298 (.in(1'b0), .out(_52), .gate(nT0));
  Pull_Resistor #(.pull(1)) pull_resistor_54 (.node(_53));
  Transistor #(.\type ("n")) transistor_299 (.in(1'b0), .out(_53), .gate(not_1_out));
  Transistor #(.\type ("n")) transistor_300 (.in(1'b0), .out(_53), .gate(IR7));
  Transistor #(.\type ("n")) transistor_301 (.in(1'b0), .out(_53), .gate(IR6));
  Transistor #(.\type ("n")) transistor_302 (.in(1'b0), .out(_53), .gate(not_8_out));
  Pull_Resistor #(.pull(1)) pull_resistor_55 (.node(_54));
  Transistor #(.\type ("n")) transistor_303 (.in(1'b0), .out(_54), .gate(nT3));
  Transistor #(.\type ("n")) transistor_304 (.in(1'b0), .out(_54), .gate(or_1_out));
  Transistor #(.\type ("n")) transistor_305 (.in(1'b0), .out(_54), .gate(IR7));
  Transistor #(.\type ("n")) transistor_306 (.in(1'b0), .out(_54), .gate(IR4));
  Transistor #(.\type ("n")) transistor_307 (.in(1'b0), .out(_54), .gate(not_5_out));
  Transistor #(.\type ("n")) transistor_308 (.in(1'b0), .out(_54), .gate(not_6_out));
  Transistor #(.\type ("n")) transistor_309 (.in(1'b0), .out(_54), .gate(not_7_out));
  Pull_Resistor #(.pull(1)) pull_resistor_56 (.node(_56));
  Pull_Resistor #(.pull(1)) pull_resistor_57 (.node(_55));
  Transistor #(.\type ("n")) transistor_310 (.in(1'b0), .out(_56), .gate(nT5));
  Transistor #(.\type ("n")) transistor_311 (.in(1'b0), .out(_55), .gate(not_1_out));
  Transistor #(.\type ("n")) transistor_312 (.in(1'b0), .out(_56), .gate(or_1_out));
  Transistor #(.\type ("n")) transistor_313 (.in(1'b0), .out(_55), .gate(IR7));
  Transistor #(.\type ("n")) transistor_314 (.in(1'b0), .out(_56), .gate(IR7));
  Transistor #(.\type ("n")) transistor_315 (.in(1'b0), .out(_56), .gate(IR4));
  Transistor #(.\type ("n")) transistor_316 (.in(1'b0), .out(_56), .gate(IR3));
  Transistor #(.\type ("n")) transistor_317 (.in(1'b0), .out(_56), .gate(IR2));
  Transistor #(.\type ("n")) transistor_318 (.in(1'b0), .out(_56), .gate(IR6));
  Transistor #(.\type ("n")) transistor_319 (.in(1'b0), .out(_55), .gate(IR6));
  Transistor #(.\type ("n")) transistor_320 (.in(1'b0), .out(_56), .gate(not_8_out));
  Pull_Resistor #(.pull(1)) pull_resistor_58 (.node(_57));
  Transistor #(.\type ("n")) transistor_321 (.in(1'b0), .out(_57), .gate(nT2));
  Transistor #(.\type ("n")) transistor_322 (.in(1'b0), .out(_57), .gate(or_1_out));
  Transistor #(.\type ("n")) transistor_323 (.in(1'b0), .out(_57), .gate(IR7));
  Transistor #(.\type ("n")) transistor_324 (.in(1'b0), .out(_57), .gate(IR4));
  Transistor #(.\type ("n")) transistor_325 (.in(1'b0), .out(_57), .gate(IR2));
  Pull_Resistor #(.pull(1)) pull_resistor_59 (.node(_58));
  Transistor #(.\type ("n")) transistor_326 (.in(1'b0), .out(_58), .gate(or_1_out));
  Transistor #(.\type ("n")) transistor_327 (.in(1'b0), .out(_58), .gate(not_3_out));
  Transistor #(.\type ("n")) transistor_328 (.in(1'b0), .out(_58), .gate(not_4_out));
  Transistor #(.\type ("n")) transistor_329 (.in(1'b0), .out(_58), .gate(not_5_out));
  Transistor #(.\type ("n")) transistor_330 (.in(1'b0), .out(_58), .gate(IR2));
  Transistor #(.\type ("n")) transistor_331 (.in(1'b0), .out(_58), .gate(IR6));
  Transistor #(.\type ("n")) transistor_332 (.in(1'b0), .out(_58), .gate(IR5));
  Transistor #(.\type ("n")) transistor_333 (.in(1'b0), .out(_58), .gate(nT0));
  Pull_Resistor #(.pull(1)) pull_resistor_60 (.node(_59));
  Pull_Resistor #(.pull(1)) pull_resistor_61 (.node(_60));
  Transistor #(.\type ("n")) transistor_334 (.in(1'b0), .out(_59), .gate(not_2_out));
  Transistor #(.\type ("n")) transistor_335 (.in(1'b0), .out(_60), .gate(not_2_out));
  Transistor #(.\type ("n")) transistor_336 (.in(1'b0), .out(_59), .gate(IR7));
  Transistor #(.\type ("n")) transistor_337 (.in(1'b0), .out(_60), .gate(not_7_out));
  Transistor #(.\type ("n")) transistor_338 (.in(1'b0), .out(_60), .gate(not_8_out));
  Transistor #(.\type ("n")) transistor_339 (.in(1'b0), .out(_60), .gate(nT1X));
  Transistor #(.\type ("n")) transistor_340 (.in(1'b0), .out(_59), .gate(nT1X));
  Pull_Resistor #(.pull(1)) pull_resistor_62 (.node(_61));
  Transistor #(.\type ("n")) transistor_341 (.in(1'b0), .out(_61), .gate(not_1_out));
  Transistor #(.\type ("n")) transistor_342 (.in(1'b0), .out(_61), .gate(IR7));
  Transistor #(.\type ("n")) transistor_343 (.in(1'b0), .out(_61), .gate(IR4));
  Transistor #(.\type ("n")) transistor_344 (.in(1'b0), .out(_61), .gate(not_5_out));
  Transistor #(.\type ("n")) transistor_345 (.in(1'b0), .out(_61), .gate(IR2));
  Transistor #(.\type ("n")) transistor_346 (.in(1'b0), .out(_61), .gate(nT1X));
  Pull_Resistor #(.pull(1)) pull_resistor_63 (.node(_62));
  Transistor #(.\type ("n")) transistor_347 (.in(1'b0), .out(_62), .gate(not_1_out));
  Transistor #(.\type ("n")) transistor_348 (.in(1'b0), .out(_62), .gate(not_3_out));
  Transistor #(.\type ("n")) transistor_349 (.in(1'b0), .out(_62), .gate(IR4));
  Transistor #(.\type ("n")) transistor_350 (.in(1'b0), .out(_62), .gate(not_5_out));
  Transistor #(.\type ("n")) transistor_351 (.in(1'b0), .out(_62), .gate(IR2));
  Transistor #(.\type ("n")) transistor_352 (.in(1'b0), .out(_62), .gate(IR6));
  Transistor #(.\type ("n")) transistor_353 (.in(1'b0), .out(_62), .gate(IR5));
  Transistor #(.\type ("n")) transistor_354 (.in(1'b0), .out(_62), .gate(nT0));
  Pull_Resistor #(.pull(1)) pull_resistor_64 (.node(_63));
  Pull_Resistor #(.pull(1)) pull_resistor_65 (.node(_64));
  Transistor #(.\type ("n")) transistor_355 (.in(1'b0), .out(_63), .gate(or_1_out));
  Transistor #(.\type ("n")) transistor_356 (.in(1'b0), .out(_64), .gate(not_2_out));
  Transistor #(.\type ("n")) transistor_357 (.in(1'b0), .out(_63), .gate(IR7));
  Transistor #(.\type ("n")) transistor_358 (.in(1'b0), .out(_64), .gate(not_3_out));
  Transistor #(.\type ("n")) transistor_359 (.in(1'b0), .out(_63), .gate(IR4));
  Transistor #(.\type ("n")) transistor_360 (.in(1'b0), .out(_63), .gate(not_5_out));
  Transistor #(.\type ("n")) transistor_361 (.in(1'b0), .out(_63), .gate(IR2));
  Transistor #(.\type ("n")) transistor_362 (.in(1'b0), .out(_64), .gate(IR6));
  Transistor #(.\type ("n")) transistor_363 (.in(1'b0), .out(_63), .gate(not_7_out));
  Transistor #(.\type ("n")) transistor_364 (.in(1'b0), .out(_63), .gate(not_8_out));
  Transistor #(.\type ("n")) transistor_365 (.in(1'b0), .out(_64), .gate(not_8_out));
  Transistor #(.\type ("n")) transistor_366 (.in(1'b0), .out(_63), .gate(nT0));
  Transistor #(.\type ("n")) transistor_367 (.in(1'b0), .out(_64), .gate(nT0));
  Pull_Resistor #(.pull(1)) pull_resistor_66 (.node(_65));
  Transistor #(.\type ("n")) transistor_368 (.in(1'b0), .out(_65), .gate(not_2_out));
  Transistor #(.\type ("n")) transistor_369 (.in(1'b0), .out(_65), .gate(nT0));
  Pull_Resistor #(.pull(1)) pull_resistor_67 (.node(_66));
  Transistor #(.\type ("n")) transistor_370 (.in(1'b0), .out(_66), .gate(or_1_out));
  Transistor #(.\type ("n")) transistor_371 (.in(1'b0), .out(_66), .gate(not_3_out));
  Transistor #(.\type ("n")) transistor_372 (.in(1'b0), .out(_66), .gate(IR4));
  Transistor #(.\type ("n")) transistor_373 (.in(1'b0), .out(_66), .gate(not_5_out));
  Transistor #(.\type ("n")) transistor_374 (.in(1'b0), .out(_66), .gate(IR2));
  Transistor #(.\type ("n")) transistor_375 (.in(1'b0), .out(_66), .gate(IR6));
  Transistor #(.\type ("n")) transistor_376 (.in(1'b0), .out(_66), .gate(not_8_out));
  Transistor #(.\type ("n")) transistor_377 (.in(1'b0), .out(_66), .gate(nT0));
  Pull_Resistor #(.pull(1)) pull_resistor_68 (.node(_68));
  Pull_Resistor #(.pull(1)) pull_resistor_69 (.node(_67));
  Transistor #(.\type ("n")) transistor_378 (.in(1'b0), .out(_68), .gate(not_1_out));
  Transistor #(.\type ("n")) transistor_379 (.in(1'b0), .out(_67), .gate(not_1_out));
  Transistor #(.\type ("n")) transistor_380 (.in(1'b0), .out(_67), .gate(IR7));
  Transistor #(.\type ("n")) transistor_381 (.in(1'b0), .out(_68), .gate(not_3_out));
  Transistor #(.\type ("n")) transistor_382 (.in(1'b0), .out(_67), .gate(IR4));
  Transistor #(.\type ("n")) transistor_383 (.in(1'b0), .out(_68), .gate(IR4));
  Transistor #(.\type ("n")) transistor_384 (.in(1'b0), .out(_67), .gate(not_5_out));
  Transistor #(.\type ("n")) transistor_385 (.in(1'b0), .out(_68), .gate(not_5_out));
  Transistor #(.\type ("n")) transistor_386 (.in(1'b0), .out(_68), .gate(IR2));
  Transistor #(.\type ("n")) transistor_387 (.in(1'b0), .out(_67), .gate(IR2));
  Transistor #(.\type ("n")) transistor_388 (.in(1'b0), .out(_68), .gate(IR6));
  Transistor #(.\type ("n")) transistor_389 (.in(1'b0), .out(_68), .gate(not_8_out));
  Transistor #(.\type ("n")) transistor_390 (.in(1'b0), .out(_67), .gate(nT0));
  Transistor #(.\type ("n")) transistor_391 (.in(1'b0), .out(_68), .gate(nT0));
  Pull_Resistor #(.pull(1)) pull_resistor_70 (.node(_69));
  Transistor #(.\type ("n")) transistor_392 (.in(1'b0), .out(_69), .gate(or_1_out));
  Transistor #(.\type ("n")) transistor_393 (.in(1'b0), .out(_69), .gate(IR7));
  Transistor #(.\type ("n")) transistor_394 (.in(1'b0), .out(_69), .gate(IR4));
  Transistor #(.\type ("n")) transistor_395 (.in(1'b0), .out(_69), .gate(not_6_out));
  Transistor #(.\type ("n")) transistor_396 (.in(1'b0), .out(_69), .gate(IR6));
  Transistor #(.\type ("n")) transistor_397 (.in(1'b0), .out(_69), .gate(not_8_out));
  Transistor #(.\type ("n")) transistor_398 (.in(1'b0), .out(_69), .gate(nT0));
  Pull_Resistor #(.pull(1)) pull_resistor_71 (.node(_70));
  Transistor #(.\type ("n")) transistor_399 (.in(1'b0), .out(_70), .gate(not_2_out));
  Transistor #(.\type ("n")) transistor_400 (.in(1'b0), .out(_70), .gate(IR7));
  Transistor #(.\type ("n")) transistor_401 (.in(1'b0), .out(_70), .gate(IR6));
  Transistor #(.\type ("n")) transistor_402 (.in(1'b0), .out(_70), .gate(not_8_out));
  Transistor #(.\type ("n")) transistor_403 (.in(1'b0), .out(_70), .gate(nT0));
  Pull_Resistor #(.pull(1)) pull_resistor_72 (.node(_72));
  Pull_Resistor #(.pull(1)) pull_resistor_73 (.node(_71));
  Transistor #(.\type ("n")) transistor_404 (.in(1'b0), .out(_72), .gate(nT5));
  Transistor #(.\type ("n")) transistor_405 (.in(1'b0), .out(_71), .gate(nT4));
  Transistor #(.\type ("n")) transistor_406 (.in(1'b0), .out(_72), .gate(not_2_out));
  Transistor #(.\type ("n")) transistor_407 (.in(1'b0), .out(_71), .gate(not_4_out));
  Transistor #(.\type ("n")) transistor_408 (.in(1'b0), .out(_72), .gate(not_4_out));
  Transistor #(.\type ("n")) transistor_409 (.in(1'b0), .out(_72), .gate(IR3));
  Transistor #(.\type ("n")) transistor_410 (.in(1'b0), .out(_71), .gate(not_5_out));
  Transistor #(.\type ("n")) transistor_411 (.in(1'b0), .out(_72), .gate(IR2));
  Pull_Resistor #(.pull(1)) pull_resistor_74 (.node(_73));
  Transistor #(.\type ("n")) transistor_412 (.in(1'b0), .out(_73), .gate(or_1_out));
  Transistor #(.\type ("n")) transistor_413 (.in(1'b0), .out(_73), .gate(not_4_out));
  Transistor #(.\type ("n")) transistor_414 (.in(1'b0), .out(_73), .gate(IR3));
  Transistor #(.\type ("n")) transistor_415 (.in(1'b0), .out(_73), .gate(IR2));
  Transistor #(.\type ("n")) transistor_416 (.in(1'b0), .out(_73), .gate(nT0));
  Pull_Resistor #(.pull(1)) pull_resistor_75 (.node(_74));
  Pull_Resistor #(.pull(1)) pull_resistor_76 (.node(_75));
  Transistor #(.\type ("n")) transistor_417 (.in(1'b0), .out(_74), .gate(nT2));
  Transistor #(.\type ("n")) transistor_418 (.in(1'b0), .out(_75), .gate(not_1_out));
  Transistor #(.\type ("n")) transistor_419 (.in(1'b0), .out(_74), .gate(or_1_out));
  Transistor #(.\type ("n")) transistor_420 (.in(1'b0), .out(_74), .gate(IR7));
  Transistor #(.\type ("n")) transistor_421 (.in(1'b0), .out(_75), .gate(IR7));
  Transistor #(.\type ("n")) transistor_422 (.in(1'b0), .out(_75), .gate(IR4));
  Transistor #(.\type ("n")) transistor_423 (.in(1'b0), .out(_74), .gate(IR4));
  Transistor #(.\type ("n")) transistor_424 (.in(1'b0), .out(_75), .gate(not_5_out));
  Transistor #(.\type ("n")) transistor_425 (.in(1'b0), .out(_74), .gate(not_5_out));
  Transistor #(.\type ("n")) transistor_426 (.in(1'b0), .out(_74), .gate(IR2));
  Transistor #(.\type ("n")) transistor_427 (.in(1'b0), .out(_75), .gate(IR2));
  Transistor #(.\type ("n")) transistor_428 (.in(1'b0), .out(_75), .gate(not_7_out));
  Transistor #(.\type ("n")) transistor_429 (.in(1'b0), .out(_74), .gate(not_7_out));
  Transistor #(.\type ("n")) transistor_430 (.in(1'b0), .out(_74), .gate(IR5));
  Transistor #(.\type ("n")) transistor_431 (.in(1'b0), .out(_75), .gate(nT0));
  Pull_Resistor #(.pull(1)) pull_resistor_77 (.node(_76));
  Transistor #(.\type ("n")) transistor_432 (.in(1'b0), .out(_76), .gate(not_1_out));
  Transistor #(.\type ("n")) transistor_433 (.in(1'b0), .out(_76), .gate(IR7));
  Transistor #(.\type ("n")) transistor_434 (.in(1'b0), .out(_76), .gate(not_7_out));
  Pull_Resistor #(.pull(1)) pull_resistor_78 (.node(_77));
  Transistor #(.\type ("n")) transistor_435 (.in(1'b0), .out(_77), .gate(nT2));
  Transistor #(.\type ("n")) transistor_436 (.in(1'b0), .out(_77), .gate(or_1_out));
  Transistor #(.\type ("n")) transistor_437 (.in(1'b0), .out(_77), .gate(IR7));
  Transistor #(.\type ("n")) transistor_438 (.in(1'b0), .out(_77), .gate(IR4));
  Transistor #(.\type ("n")) transistor_439 (.in(1'b0), .out(_77), .gate(IR3));
  Transistor #(.\type ("n")) transistor_440 (.in(1'b0), .out(_77), .gate(IR2));
  Transistor #(.\type ("n")) transistor_441 (.in(1'b0), .out(_77), .gate(IR6));
  Transistor #(.\type ("n")) transistor_442 (.in(1'b0), .out(_77), .gate(IR5));
  Pull_Resistor #(.pull(1)) pull_resistor_79 (.node(_79));
  Pull_Resistor #(.pull(1)) pull_resistor_80 (.node(_78));
  Transistor #(.\type ("n")) transistor_443 (.in(1'b0), .out(_78), .gate(nT3));
  Transistor #(.\type ("n")) transistor_444 (.in(1'b0), .out(_78), .gate(or_1_out));
  Transistor #(.\type ("n")) transistor_445 (.in(1'b0), .out(_79), .gate(not_2_out));
  Transistor #(.\type ("n")) transistor_446 (.in(1'b0), .out(_78), .gate(IR7));
  Transistor #(.\type ("n")) transistor_447 (.in(1'b0), .out(_79), .gate(not_3_out));
  Transistor #(.\type ("n")) transistor_448 (.in(1'b0), .out(_78), .gate(IR4));
  Transistor #(.\type ("n")) transistor_449 (.in(1'b0), .out(_78), .gate(IR3));
  Transistor #(.\type ("n")) transistor_450 (.in(1'b0), .out(_78), .gate(IR2));
  Transistor #(.\type ("n")) transistor_451 (.in(1'b0), .out(_78), .gate(IR6));
  Transistor #(.\type ("n")) transistor_452 (.in(1'b0), .out(_79), .gate(IR6));
  Transistor #(.\type ("n")) transistor_453 (.in(1'b0), .out(_79), .gate(IR5));
  Transistor #(.\type ("n")) transistor_454 (.in(1'b0), .out(_78), .gate(not_8_out));
  Pull_Resistor #(.pull(1)) pull_resistor_81 (.node(_80));
  Transistor #(.\type ("n")) transistor_455 (.in(1'b0), .out(_80), .gate(nT2));
  Transistor #(.\type ("n")) transistor_456 (.in(1'b0), .out(_80), .gate(or_1_out));
  Transistor #(.\type ("n")) transistor_457 (.in(1'b0), .out(_80), .gate(not_4_out));
  Transistor #(.\type ("n")) transistor_458 (.in(1'b0), .out(_80), .gate(IR3));
  Transistor #(.\type ("n")) transistor_459 (.in(1'b0), .out(_80), .gate(IR2));
  Pull_Resistor #(.pull(1)) pull_resistor_82 (.node(_81));
  Transistor #(.\type ("n")) transistor_460 (.in(1'b0), .out(_81), .gate(nT2));
  Transistor #(.\type ("n")) transistor_461 (.in(1'b0), .out(_81), .gate(IR3));
  Transistor #(.\type ("n")) transistor_462 (.in(1'b0), .out(_81), .gate(not_6_out));
  Pull_Resistor #(.pull(1)) pull_resistor_83 (.node(_83));
  Pull_Resistor #(.pull(1)) pull_resistor_84 (.node(_82));
  Transistor #(.\type ("n")) transistor_463 (.in(1'b0), .out(_83), .gate(nT2));
  Transistor #(.\type ("n")) transistor_464 (.in(1'b0), .out(_82), .gate(nT2));
  Transistor #(.\type ("n")) transistor_465 (.in(1'b0), .out(_82), .gate(not_2_out));
  Transistor #(.\type ("n")) transistor_466 (.in(1'b0), .out(_82), .gate(IR3));
  Transistor #(.\type ("n")) transistor_467 (.in(1'b0), .out(_83), .gate(not_5_out));
  Transistor #(.\type ("n")) transistor_468 (.in(1'b0), .out(_82), .gate(IR2));
  Pull_Resistor #(.pull(1)) pull_resistor_85 (.node(_84));
  Transistor #(.\type ("n")) transistor_469 (.in(1'b0), .out(_84), .gate(nT5));
  Transistor #(.\type ("n")) transistor_470 (.in(1'b0), .out(_84), .gate(or_1_out));
  Transistor #(.\type ("n")) transistor_471 (.in(1'b0), .out(_84), .gate(IR7));
  Transistor #(.\type ("n")) transistor_472 (.in(1'b0), .out(_84), .gate(IR4));
  Transistor #(.\type ("n")) transistor_473 (.in(1'b0), .out(_84), .gate(IR3));
  Transistor #(.\type ("n")) transistor_474 (.in(1'b0), .out(_84), .gate(IR2));
  Transistor #(.\type ("n")) transistor_475 (.in(1'b0), .out(_84), .gate(not_7_out));
  Transistor #(.\type ("n")) transistor_476 (.in(1'b0), .out(_84), .gate(not_8_out));
  Pull_Resistor #(.pull(1)) pull_resistor_86 (.node(_85));
  Transistor #(.\type ("n")) transistor_477 (.in(1'b0), .out(_85), .gate(nT4));
  Pull_Resistor #(.pull(1)) pull_resistor_87 (.node(_87));
  Pull_Resistor #(.pull(1)) pull_resistor_88 (.node(_86));
  Transistor #(.\type ("n")) transistor_478 (.in(1'b0), .out(_86), .gate(nT3));
  Transistor #(.\type ("n")) transistor_479 (.in(1'b0), .out(_87), .gate(or_1_out));
  Transistor #(.\type ("n")) transistor_480 (.in(1'b0), .out(_87), .gate(IR7));
  Transistor #(.\type ("n")) transistor_481 (.in(1'b0), .out(_87), .gate(IR4));
  Transistor #(.\type ("n")) transistor_482 (.in(1'b0), .out(_87), .gate(IR3));
  Transistor #(.\type ("n")) transistor_483 (.in(1'b0), .out(_87), .gate(IR2));
  Transistor #(.\type ("n")) transistor_484 (.in(1'b0), .out(_87), .gate(IR5));
  Transistor #(.\type ("n")) transistor_485 (.in(1'b0), .out(_87), .gate(nT0));
  Pull_Resistor #(.pull(1)) pull_resistor_89 (.node(_88));
  Transistor #(.\type ("n")) transistor_486 (.in(1'b0), .out(_88), .gate(or_1_out));
  Transistor #(.\type ("n")) transistor_487 (.in(1'b0), .out(_88), .gate(IR7));
  Transistor #(.\type ("n")) transistor_488 (.in(1'b0), .out(_88), .gate(IR4));
  Transistor #(.\type ("n")) transistor_489 (.in(1'b0), .out(_88), .gate(not_5_out));
  Transistor #(.\type ("n")) transistor_490 (.in(1'b0), .out(_88), .gate(not_6_out));
  Transistor #(.\type ("n")) transistor_491 (.in(1'b0), .out(_88), .gate(not_7_out));
  Transistor #(.\type ("n")) transistor_492 (.in(1'b0), .out(_88), .gate(nT0));
  Pull_Resistor #(.pull(1)) pull_resistor_90 (.node(_89));
  Transistor #(.\type ("n")) transistor_493 (.in(1'b0), .out(_89), .gate(nT5));
  Transistor #(.\type ("n")) transistor_494 (.in(1'b0), .out(_89), .gate(not_2_out));
  Transistor #(.\type ("n")) transistor_495 (.in(1'b0), .out(_89), .gate(IR4));
  Transistor #(.\type ("n")) transistor_496 (.in(1'b0), .out(_89), .gate(IR3));
  Transistor #(.\type ("n")) transistor_497 (.in(1'b0), .out(_89), .gate(IR2));
  Pull_Resistor #(.pull(1)) pull_resistor_91 (.node(_90));
  Transistor #(.\type ("n")) transistor_498 (.in(1'b0), .out(_90), .gate(nT3));
  Transistor #(.\type ("n")) transistor_499 (.in(1'b0), .out(_90), .gate(not_5_out));
  Pull_Resistor #(.pull(1)) pull_resistor_92 (.node(_91));
  Transistor #(.\type ("n")) transistor_500 (.in(1'b0), .out(_91), .gate(nT4));
  Transistor #(.\type ("n")) transistor_501 (.in(1'b0), .out(_91), .gate(not_2_out));
  Transistor #(.\type ("n")) transistor_502 (.in(1'b0), .out(_91), .gate(not_4_out));
  Transistor #(.\type ("n")) transistor_503 (.in(1'b0), .out(_91), .gate(IR3));
  Transistor #(.\type ("n")) transistor_504 (.in(1'b0), .out(_91), .gate(IR2));
  Pull_Resistor #(.pull(1)) pull_resistor_93 (.node(_92));
  Transistor #(.\type ("n")) transistor_505 (.in(1'b0), .out(_92), .gate(nT3));
  Transistor #(.\type ("n")) transistor_506 (.in(1'b0), .out(_92), .gate(not_4_out));
  Transistor #(.\type ("n")) transistor_507 (.in(1'b0), .out(_92), .gate(not_5_out));
  Pull_Resistor #(.pull(1)) pull_resistor_94 (.node(_94));
  Pull_Resistor #(.pull(1)) pull_resistor_95 (.node(_93));
  Transistor #(.\type ("n")) transistor_508 (.in(1'b0), .out(_93), .gate(nT3));
  Transistor #(.\type ("n")) transistor_509 (.in(1'b0), .out(_93), .gate(or_1_out));
  Transistor #(.\type ("n")) transistor_510 (.in(1'b0), .out(_94), .gate(or_1_out));
  Transistor #(.\type ("n")) transistor_511 (.in(1'b0), .out(_94), .gate(IR7));
  Transistor #(.\type ("n")) transistor_512 (.in(1'b0), .out(_94), .gate(IR4));
  Transistor #(.\type ("n")) transistor_513 (.in(1'b0), .out(_93), .gate(not_4_out));
  Transistor #(.\type ("n")) transistor_514 (.in(1'b0), .out(_94), .gate(IR3));
  Transistor #(.\type ("n")) transistor_515 (.in(1'b0), .out(_93), .gate(IR3));
  Transistor #(.\type ("n")) transistor_516 (.in(1'b0), .out(_94), .gate(IR2));
  Transistor #(.\type ("n")) transistor_517 (.in(1'b0), .out(_93), .gate(IR2));
  Transistor #(.\type ("n")) transistor_518 (.in(1'b0), .out(_94), .gate(IR5));
  Pull_Resistor #(.pull(1)) pull_resistor_96 (.node(_95));
  Transistor #(.\type ("n")) transistor_519 (.in(1'b0), .out(_95), .gate(or_1_out));
  Transistor #(.\type ("n")) transistor_520 (.in(1'b0), .out(_95), .gate(IR7));
  Transistor #(.\type ("n")) transistor_521 (.in(1'b0), .out(_95), .gate(IR4));
  Transistor #(.\type ("n")) transistor_522 (.in(1'b0), .out(_95), .gate(IR3));
  Transistor #(.\type ("n")) transistor_523 (.in(1'b0), .out(_95), .gate(IR2));
  Transistor #(.\type ("n")) transistor_524 (.in(1'b0), .out(_95), .gate(IR6));
  Transistor #(.\type ("n")) transistor_525 (.in(1'b0), .out(_95), .gate(not_8_out));
  Pull_Resistor #(.pull(1)) pull_resistor_97 (.node(_96));
  Transistor #(.\type ("n")) transistor_526 (.in(1'b0), .out(_96), .gate(or_1_out));
  Transistor #(.\type ("n")) transistor_527 (.in(1'b0), .out(_96), .gate(IR7));
  Transistor #(.\type ("n")) transistor_528 (.in(1'b0), .out(_96), .gate(IR4));
  Transistor #(.\type ("n")) transistor_529 (.in(1'b0), .out(_96), .gate(not_5_out));
  Transistor #(.\type ("n")) transistor_530 (.in(1'b0), .out(_96), .gate(not_6_out));
  Transistor #(.\type ("n")) transistor_531 (.in(1'b0), .out(_96), .gate(not_7_out));
  Pull_Resistor #(.pull(1)) pull_resistor_98 (.node(_97));
  Transistor #(.\type ("n")) transistor_532 (.in(1'b0), .out(_97), .gate(not_3_out));
  Transistor #(.\type ("n")) transistor_533 (.in(1'b0), .out(_97), .gate(IR6));
  Transistor #(.\type ("n")) transistor_534 (.in(1'b0), .out(_97), .gate(IR5));
  Pull_Resistor #(.pull(1)) pull_resistor_99 (.node(_98));
  Transistor #(.\type ("n")) transistor_535 (.in(1'b0), .out(_98), .gate(nT4));
  Transistor #(.\type ("n")) transistor_536 (.in(1'b0), .out(_98), .gate(or_1_out));
  Transistor #(.\type ("n")) transistor_537 (.in(1'b0), .out(_98), .gate(IR7));
  Transistor #(.\type ("n")) transistor_538 (.in(1'b0), .out(_98), .gate(IR4));
  Transistor #(.\type ("n")) transistor_539 (.in(1'b0), .out(_98), .gate(IR3));
  Transistor #(.\type ("n")) transistor_540 (.in(1'b0), .out(_98), .gate(IR2));
  Transistor #(.\type ("n")) transistor_541 (.in(1'b0), .out(_98), .gate(IR6));
  Transistor #(.\type ("n")) transistor_542 (.in(1'b0), .out(_98), .gate(IR5));
  Pull_Resistor #(.pull(1)) pull_resistor_100 (.node(_100));
  Pull_Resistor #(.pull(1)) pull_resistor_101 (.node(_99));
  Transistor #(.\type ("n")) transistor_543 (.in(1'b0), .out(_100), .gate(nT2));
  Transistor #(.\type ("n")) transistor_544 (.in(1'b0), .out(_99), .gate(nT2));
  Transistor #(.\type ("n")) transistor_545 (.in(1'b0), .out(_99), .gate(or_1_out));
  Transistor #(.\type ("n")) transistor_546 (.in(1'b0), .out(_100), .gate(or_1_out));
  Transistor #(.\type ("n")) transistor_547 (.in(1'b0), .out(_100), .gate(IR7));
  Transistor #(.\type ("n")) transistor_548 (.in(1'b0), .out(_99), .gate(IR7));
  Transistor #(.\type ("n")) transistor_549 (.in(1'b0), .out(_100), .gate(IR4));
  Transistor #(.\type ("n")) transistor_550 (.in(1'b0), .out(_99), .gate(IR4));
  Transistor #(.\type ("n")) transistor_551 (.in(1'b0), .out(_100), .gate(not_5_out));
  Transistor #(.\type ("n")) transistor_552 (.in(1'b0), .out(_99), .gate(not_5_out));
  Transistor #(.\type ("n")) transistor_553 (.in(1'b0), .out(_100), .gate(IR2));
  Transistor #(.\type ("n")) transistor_554 (.in(1'b0), .out(_99), .gate(IR2));
  Transistor #(.\type ("n")) transistor_555 (.in(1'b0), .out(_99), .gate(IR6));
  Transistor #(.\type ("n")) transistor_556 (.in(1'b0), .out(_100), .gate(IR5));
  Transistor #(.\type ("n")) transistor_557 (.in(1'b0), .out(_99), .gate(IR5));
  Pull_Resistor #(.pull(1)) pull_resistor_102 (.node(_101));
  Transistor #(.\type ("n")) transistor_558 (.in(1'b0), .out(_101), .gate(nT4));
  Transistor #(.\type ("n")) transistor_559 (.in(1'b0), .out(_101), .gate(or_1_out));
  Transistor #(.\type ("n")) transistor_560 (.in(1'b0), .out(_101), .gate(IR7));
  Transistor #(.\type ("n")) transistor_561 (.in(1'b0), .out(_101), .gate(IR4));
  Transistor #(.\type ("n")) transistor_562 (.in(1'b0), .out(_101), .gate(not_5_out));
  Transistor #(.\type ("n")) transistor_563 (.in(1'b0), .out(_101), .gate(not_6_out));
  Transistor #(.\type ("n")) transistor_564 (.in(1'b0), .out(_101), .gate(not_7_out));
  Pull_Resistor #(.pull(1)) pull_resistor_103 (.node(_102));
  Transistor #(.\type ("n")) transistor_565 (.in(1'b0), .out(_102), .gate(nT5));
  Transistor #(.\type ("n")) transistor_566 (.in(1'b0), .out(_102), .gate(or_1_out));
  Transistor #(.\type ("n")) transistor_567 (.in(1'b0), .out(_102), .gate(IR7));
  Transistor #(.\type ("n")) transistor_568 (.in(1'b0), .out(_102), .gate(IR4));
  Transistor #(.\type ("n")) transistor_569 (.in(1'b0), .out(_102), .gate(IR3));
  Transistor #(.\type ("n")) transistor_570 (.in(1'b0), .out(_102), .gate(IR2));
  Transistor #(.\type ("n")) transistor_571 (.in(1'b0), .out(_102), .gate(not_7_out));
  Pull_Resistor #(.pull(1)) pull_resistor_104 (.node(_103));
  Transistor #(.\type ("n")) transistor_572 (.in(1'b0), .out(_103), .gate(nT5));
  Transistor #(.\type ("n")) transistor_573 (.in(1'b0), .out(_103), .gate(or_1_out));
  Transistor #(.\type ("n")) transistor_574 (.in(1'b0), .out(_103), .gate(IR7));
  Transistor #(.\type ("n")) transistor_575 (.in(1'b0), .out(_103), .gate(IR4));
  Transistor #(.\type ("n")) transistor_576 (.in(1'b0), .out(_103), .gate(IR3));
  Transistor #(.\type ("n")) transistor_577 (.in(1'b0), .out(_103), .gate(IR2));
  Transistor #(.\type ("n")) transistor_578 (.in(1'b0), .out(_103), .gate(IR6));
  Transistor #(.\type ("n")) transistor_579 (.in(1'b0), .out(_103), .gate(not_8_out));
  Pull_Resistor #(.pull(1)) pull_resistor_105 (.node(_104));
  Pull_Resistor #(.pull(1)) pull_resistor_106 (.node(_105));
  Transistor #(.\type ("n")) transistor_580 (.in(1'b0), .out(_105), .gate(nT3));
  Transistor #(.\type ("n")) transistor_581 (.in(1'b0), .out(_104), .gate(nT2));
  Transistor #(.\type ("n")) transistor_582 (.in(1'b0), .out(_105), .gate(or_1_out));
  Transistor #(.\type ("n")) transistor_583 (.in(1'b0), .out(_104), .gate(or_1_out));
  Transistor #(.\type ("n")) transistor_584 (.in(1'b0), .out(_104), .gate(IR7));
  Transistor #(.\type ("n")) transistor_585 (.in(1'b0), .out(_105), .gate(IR7));
  Transistor #(.\type ("n")) transistor_586 (.in(1'b0), .out(_105), .gate(IR4));
  Transistor #(.\type ("n")) transistor_587 (.in(1'b0), .out(_104), .gate(IR4));
  Transistor #(.\type ("n")) transistor_588 (.in(1'b0), .out(_105), .gate(not_5_out));
  Transistor #(.\type ("n")) transistor_589 (.in(1'b0), .out(_104), .gate(not_5_out));
  Transistor #(.\type ("n")) transistor_590 (.in(1'b0), .out(_105), .gate(IR2));
  Transistor #(.\type ("n")) transistor_591 (.in(1'b0), .out(_104), .gate(not_6_out));
  Transistor #(.\type ("n")) transistor_592 (.in(1'b0), .out(_104), .gate(not_7_out));
  Transistor #(.\type ("n")) transistor_593 (.in(1'b0), .out(_104), .gate(IR5));
  Transistor #(.\type ("n")) transistor_594 (.in(1'b0), .out(_105), .gate(not_8_out));
  Pull_Resistor #(.pull(1)) pull_resistor_107 (.node(_106));
  Transistor #(.\type ("n")) transistor_595 (.in(1'b0), .out(_106), .gate(not_1_out));
  Transistor #(.\type ("n")) transistor_596 (.in(1'b0), .out(_106), .gate(not_7_out));
  Pull_Resistor #(.pull(1)) pull_resistor_108 (.node(_107));
  Transistor #(.\type ("n")) transistor_597 (.in(1'b0), .out(_107), .gate(not_1_out));
  Transistor #(.\type ("n")) transistor_598 (.in(1'b0), .out(_107), .gate(IR7));
  Transistor #(.\type ("n")) transistor_599 (.in(1'b0), .out(_107), .gate(IR6));
  Pull_Resistor #(.pull(1)) pull_resistor_109 (.node(_108));
  Transistor #(.\type ("n")) transistor_600 (.in(1'b0), .out(_108), .gate(or_1_out));
  Transistor #(.\type ("n")) transistor_601 (.in(1'b0), .out(_108), .gate(IR7));
  Transistor #(.\type ("n")) transistor_602 (.in(1'b0), .out(_108), .gate(not_4_out));
  Transistor #(.\type ("n")) transistor_603 (.in(1'b0), .out(_108), .gate(not_5_out));
  Transistor #(.\type ("n")) transistor_604 (.in(1'b0), .out(_108), .gate(IR2));
  Transistor #(.\type ("n")) transistor_605 (.in(1'b0), .out(_108), .gate(not_7_out));
  Transistor #(.\type ("n")) transistor_606 (.in(1'b0), .out(_108), .gate(nT0));
  Pull_Resistor #(.pull(1)) pull_resistor_110 (.node(_109));
  Transistor #(.\type ("n")) transistor_607 (.in(1'b0), .out(_109), .gate(or_1_out));
  Transistor #(.\type ("n")) transistor_608 (.in(1'b0), .out(_109), .gate(IR7));
  Transistor #(.\type ("n")) transistor_609 (.in(1'b0), .out(_109), .gate(IR4));
  Transistor #(.\type ("n")) transistor_610 (.in(1'b0), .out(_109), .gate(not_6_out));
  Transistor #(.\type ("n")) transistor_611 (.in(1'b0), .out(_109), .gate(IR6));
  Transistor #(.\type ("n")) transistor_612 (.in(1'b0), .out(_109), .gate(not_8_out));
  Transistor #(.\type ("n")) transistor_613 (.in(1'b0), .out(_109), .gate(nT1X));
  Pull_Resistor #(.pull(1)) pull_resistor_111 (.node(_111));
  Pull_Resistor #(.pull(1)) pull_resistor_112 (.node(_110));
  Transistor #(.\type ("n")) transistor_614 (.in(1'b0), .out(_111), .gate(nT3));
  Transistor #(.\type ("n")) transistor_615 (.in(1'b0), .out(_110), .gate(or_1_out));
  Transistor #(.\type ("n")) transistor_616 (.in(1'b0), .out(_110), .gate(IR7));
  Transistor #(.\type ("n")) transistor_617 (.in(1'b0), .out(_111), .gate(not_4_out));
  Transistor #(.\type ("n")) transistor_618 (.in(1'b0), .out(_110), .gate(not_4_out));
  Transistor #(.\type ("n")) transistor_619 (.in(1'b0), .out(_111), .gate(IR3));
  Transistor #(.\type ("n")) transistor_620 (.in(1'b0), .out(_110), .gate(not_5_out));
  Transistor #(.\type ("n")) transistor_621 (.in(1'b0), .out(_110), .gate(IR2));
  Transistor #(.\type ("n")) transistor_622 (.in(1'b0), .out(_111), .gate(not_6_out));
  Transistor #(.\type ("n")) transistor_623 (.in(1'b0), .out(_110), .gate(IR6));
  Transistor #(.\type ("n")) transistor_624 (.in(1'b0), .out(_110), .gate(nT0));
  Pull_Resistor #(.pull(1)) pull_resistor_113 (.node(_112));
  Transistor #(.\type ("n")) transistor_625 (.in(1'b0), .out(_112), .gate(not_2_out));
  Transistor #(.\type ("n")) transistor_626 (.in(1'b0), .out(_112), .gate(not_7_out));
  Transistor #(.\type ("n")) transistor_627 (.in(1'b0), .out(_112), .gate(not_8_out));
  Transistor #(.\type ("n")) transistor_628 (.in(1'b0), .out(_112), .gate(nT1X));
  Pull_Resistor #(.pull(1)) pull_resistor_114 (.node(_113));
  Transistor #(.\type ("n")) transistor_629 (.in(1'b0), .out(_113), .gate(or_1_out));
  Transistor #(.\type ("n")) transistor_630 (.in(1'b0), .out(_113), .gate(IR7));
  Transistor #(.\type ("n")) transistor_631 (.in(1'b0), .out(_113), .gate(IR4));
  Transistor #(.\type ("n")) transistor_632 (.in(1'b0), .out(_113), .gate(not_6_out));
  Transistor #(.\type ("n")) transistor_633 (.in(1'b0), .out(_113), .gate(IR6));
  Transistor #(.\type ("n")) transistor_634 (.in(1'b0), .out(_113), .gate(not_8_out));
  Transistor #(.\type ("n")) transistor_635 (.in(1'b0), .out(_113), .gate(nT0));
  Pull_Resistor #(.pull(1)) pull_resistor_115 (.node(_114));
  Pull_Resistor #(.pull(1)) pull_resistor_116 (.node(_115));
  Transistor #(.\type ("n")) transistor_636 (.in(1'b0), .out(_115), .gate(nT4));
  Transistor #(.\type ("n")) transistor_637 (.in(1'b0), .out(_114), .gate(or_1_out));
  Transistor #(.\type ("n")) transistor_638 (.in(1'b0), .out(_115), .gate(or_1_out));
  Transistor #(.\type ("n")) transistor_639 (.in(1'b0), .out(_114), .gate(IR7));
  Transistor #(.\type ("n")) transistor_640 (.in(1'b0), .out(_115), .gate(IR7));
  Transistor #(.\type ("n")) transistor_641 (.in(1'b0), .out(_114), .gate(IR4));
  Transistor #(.\type ("n")) transistor_642 (.in(1'b0), .out(_115), .gate(IR4));
  Transistor #(.\type ("n")) transistor_643 (.in(1'b0), .out(_115), .gate(IR3));
  Transistor #(.\type ("n")) transistor_644 (.in(1'b0), .out(_114), .gate(not_5_out));
  Transistor #(.\type ("n")) transistor_645 (.in(1'b0), .out(_115), .gate(IR2));
  Transistor #(.\type ("n")) transistor_646 (.in(1'b0), .out(_114), .gate(IR2));
  Transistor #(.\type ("n")) transistor_647 (.in(1'b0), .out(_114), .gate(IR6));
  Transistor #(.\type ("n")) transistor_648 (.in(1'b0), .out(_115), .gate(not_7_out));
  Transistor #(.\type ("n")) transistor_649 (.in(1'b0), .out(_115), .gate(IR5));
  Transistor #(.\type ("n")) transistor_650 (.in(1'b0), .out(_114), .gate(not_8_out));
  Transistor #(.\type ("n")) transistor_651 (.in(1'b0), .out(_114), .gate(nT0));
  Pull_Resistor #(.pull(1)) pull_resistor_117 (.node(_116));
  Transistor #(.\type ("n")) transistor_652 (.in(1'b0), .out(_116), .gate(not_2_out));
  Transistor #(.\type ("n")) transistor_653 (.in(1'b0), .out(_116), .gate(not_3_out));
  Transistor #(.\type ("n")) transistor_654 (.in(1'b0), .out(_116), .gate(not_7_out));
  Transistor #(.\type ("n")) transistor_655 (.in(1'b0), .out(_116), .gate(IR5));
  Transistor #(.\type ("n")) transistor_656 (.in(1'b0), .out(_116), .gate(nT1X));
  Pull_Resistor #(.pull(1)) pull_resistor_118 (.node(_117));
  Transistor #(.\type ("n")) transistor_657 (.in(1'b0), .out(_117), .gate(or_1_out));
  Transistor #(.\type ("n")) transistor_658 (.in(1'b0), .out(_117), .gate(not_3_out));
  Transistor #(.\type ("n")) transistor_659 (.in(1'b0), .out(_117), .gate(IR4));
  Transistor #(.\type ("n")) transistor_660 (.in(1'b0), .out(_117), .gate(not_5_out));
  Transistor #(.\type ("n")) transistor_661 (.in(1'b0), .out(_117), .gate(not_6_out));
  Transistor #(.\type ("n")) transistor_662 (.in(1'b0), .out(_117), .gate(not_7_out));
  Transistor #(.\type ("n")) transistor_663 (.in(1'b0), .out(_117), .gate(nT1X));
  Pull_Resistor #(.pull(1)) pull_resistor_119 (.node(_118));
  Pull_Resistor #(.pull(1)) pull_resistor_120 (.node(_119));
  Transistor #(.\type ("n")) transistor_664 (.in(1'b0), .out(_118), .gate(not_1_out));
  Transistor #(.\type ("n")) transistor_665 (.in(1'b0), .out(_119), .gate(or_1_out));
  Transistor #(.\type ("n")) transistor_666 (.in(1'b0), .out(_118), .gate(IR7));
  Transistor #(.\type ("n")) transistor_667 (.in(1'b0), .out(_119), .gate(not_3_out));
  Transistor #(.\type ("n")) transistor_668 (.in(1'b0), .out(_119), .gate(IR4));
  Transistor #(.\type ("n")) transistor_669 (.in(1'b0), .out(_118), .gate(IR4));
  Transistor #(.\type ("n")) transistor_670 (.in(1'b0), .out(_119), .gate(IR3));
  Transistor #(.\type ("n")) transistor_671 (.in(1'b0), .out(_118), .gate(not_5_out));
  Transistor #(.\type ("n")) transistor_672 (.in(1'b0), .out(_118), .gate(IR2));
  Transistor #(.\type ("n")) transistor_673 (.in(1'b0), .out(_118), .gate(IR6));
  Transistor #(.\type ("n")) transistor_674 (.in(1'b0), .out(_119), .gate(not_7_out));
  Transistor #(.\type ("n")) transistor_675 (.in(1'b0), .out(_119), .gate(nT1X));
  Transistor #(.\type ("n")) transistor_676 (.in(1'b0), .out(_118), .gate(nT1X));
  Pull_Resistor #(.pull(1)) pull_resistor_121 (.node(_120));
  Pull_Resistor #(.pull(1)) pull_resistor_122 (.node(_121));
  Transistor #(.\type ("n")) transistor_677 (.in(1'b0), .out(_120), .gate(or_1_out));
  Transistor #(.\type ("n")) transistor_678 (.in(1'b0), .out(_120), .gate(not_3_out));
  Transistor #(.\type ("n")) transistor_679 (.in(1'b0), .out(_120), .gate(not_4_out));
  Transistor #(.\type ("n")) transistor_680 (.in(1'b0), .out(_120), .gate(not_5_out));
  Transistor #(.\type ("n")) transistor_681 (.in(1'b0), .out(_120), .gate(IR2));
  Transistor #(.\type ("n")) transistor_682 (.in(1'b0), .out(_121), .gate(IR6));
  Transistor #(.\type ("n")) transistor_683 (.in(1'b0), .out(_120), .gate(not_7_out));
  Transistor #(.\type ("n")) transistor_684 (.in(1'b0), .out(_120), .gate(nT0));
  Pull_Resistor #(.pull(1)) pull_resistor_123 (.node(_122));
  Transistor #(.\type ("n")) transistor_685 (.in(1'b0), .out(_122), .gate(nT3));
  Transistor #(.\type ("n")) transistor_686 (.in(1'b0), .out(_122), .gate(IR4));
  Transistor #(.\type ("n")) transistor_687 (.in(1'b0), .out(_122), .gate(not_5_out));
  Transistor #(.\type ("n")) transistor_688 (.in(1'b0), .out(_122), .gate(not_6_out));
  Pull_Resistor #(.pull(1)) pull_resistor_124 (.node(_123));
  Transistor #(.\type ("n")) transistor_689 (.in(1'b0), .out(_123), .gate(nT2));
  Transistor #(.\type ("n")) transistor_690 (.in(1'b0), .out(_123), .gate(IR4));
  Transistor #(.\type ("n")) transistor_691 (.in(1'b0), .out(_123), .gate(IR3));
  Transistor #(.\type ("n")) transistor_692 (.in(1'b0), .out(_123), .gate(not_6_out));
  Pull_Resistor #(.pull(1)) pull_resistor_125 (.node(_124));
  Pull_Resistor #(.pull(1)) pull_resistor_126 (.node(_125));
  Transistor #(.\type ("n")) transistor_693 (.in(1'b0), .out(_124), .gate(nT5));
  Transistor #(.\type ("n")) transistor_694 (.in(1'b0), .out(_125), .gate(nT4));
  Transistor #(.\type ("n")) transistor_695 (.in(1'b0), .out(_124), .gate(not_2_out));
  Transistor #(.\type ("n")) transistor_696 (.in(1'b0), .out(_125), .gate(not_4_out));
  Transistor #(.\type ("n")) transistor_697 (.in(1'b0), .out(_124), .gate(IR3));
  Transistor #(.\type ("n")) transistor_698 (.in(1'b0), .out(_125), .gate(not_5_out));
  Transistor #(.\type ("n")) transistor_699 (.in(1'b0), .out(_124), .gate(IR2));
  Pull_Resistor #(.pull(1)) pull_resistor_127 (.node(_126));
  Transistor #(.\type ("n")) transistor_700 (.in(1'b0), .out(_126), .gate(IR7));
  Pull_Resistor #(.pull(1)) pull_resistor_128 (.node(_127));
  Transistor #(.\type ("n")) transistor_701 (.in(1'b0), .out(_127), .gate(or_1_out));
  Transistor #(.\type ("n")) transistor_702 (.in(1'b0), .out(_127), .gate(not_3_out));
  Transistor #(.\type ("n")) transistor_703 (.in(1'b0), .out(_127), .gate(not_4_out));
  Transistor #(.\type ("n")) transistor_704 (.in(1'b0), .out(_127), .gate(not_5_out));
  Transistor #(.\type ("n")) transistor_705 (.in(1'b0), .out(_127), .gate(IR2));
  Transistor #(.\type ("n")) transistor_706 (.in(1'b0), .out(_127), .gate(IR6));
  Transistor #(.\type ("n")) transistor_707 (.in(1'b0), .out(_127), .gate(not_8_out));
  Pull_Resistor #(.pull(1)) pull_resistor_129 (.node(_129));
  Pull_Resistor #(.pull(1)) pull_resistor_130 (.node(_128));
  Transistor #(.\type ("n")) transistor_708 (.in(1'b0), .out(_128), .gate(IR0));
  Transistor #(.\type ("n")) transistor_709 (.in(1'b0), .out(_129), .gate(or_1_out));
  Transistor #(.\type ("n")) transistor_710 (.in(1'b0), .out(_129), .gate(IR7));
  Transistor #(.\type ("n")) transistor_711 (.in(1'b0), .out(_129), .gate(IR4));
  Transistor #(.\type ("n")) transistor_712 (.in(1'b0), .out(_129), .gate(not_5_out));
  Transistor #(.\type ("n")) transistor_713 (.in(1'b0), .out(_128), .gate(not_5_out));
  Transistor #(.\type ("n")) transistor_714 (.in(1'b0), .out(_128), .gate(IR2));
  Transistor #(.\type ("n")) transistor_715 (.in(1'b0), .out(_129), .gate(IR2));

  // Notes on the sheet:
  //   TODO: Move IR0 to random logic
endmodule

module PREDECODE (
  input  PHI2,
  input  _0_IR,
  input  D0,
  input  D1,
  input  D2,
  input  D3,
  input  D4,
  input  D5,
  input  D6,
  input  D7,
  output nIMPLIED,
  output nTWOCYCLE,
  output nPD0,
  output nPD1,
  output nPD2,
  output nPD3,
  output nPD4,
  output nPD5,
  output nPD6,
  output nPD7
);

  wire d_latch_1_q, d_latch_2_q, d_latch_3_q, d_latch_4_q, d_latch_5_q, d_latch_6_q, d_latch_7_q,
       d_latch_8_q, nand1_out, nor1_out, nor2_out, nor3_out, nor4_out, nor5_out, nor_1_out, nor_2_out,
       nor_3_out, nor_4_out, nor_5_out, nor_6_out, nor_7_out, nor_8_out, not_1_out, not_2_out, not_3_out,
       not_4_out, not_5_out, not_6_out, not_7_out, not_8_out, not_9_out, not_10_out, not_11_out, not_12_out,
       not_21_out;

  not not_1 (not_1_out, D0);
  not not_2 (not_2_out, D1);
  not not_3 (not_3_out, D2);
  not not_4 (not_4_out, D3);
  not not_5 (not_5_out, D4);
  not not_6 (not_6_out, D5);
  not not_7 (not_7_out, D6);
  not not_8 (not_8_out, D7);
  D_Latch d_latch_1 (.EN(PHI2), .D(not_1_out), .Q(d_latch_1_q));  // open: NOT_Q
  D_Latch d_latch_2 (.EN(PHI2), .D(not_2_out), .Q(d_latch_2_q));  // open: NOT_Q
  D_Latch d_latch_3 (.EN(PHI2), .D(not_3_out), .Q(d_latch_3_q));  // open: NOT_Q
  D_Latch d_latch_4 (.EN(PHI2), .D(not_4_out), .Q(d_latch_4_q));  // open: NOT_Q
  D_Latch d_latch_5 (.EN(PHI2), .D(not_5_out), .Q(d_latch_5_q));  // open: NOT_Q
  D_Latch d_latch_6 (.EN(PHI2), .D(not_6_out), .Q(d_latch_6_q));  // open: NOT_Q
  D_Latch d_latch_7 (.EN(PHI2), .D(not_7_out), .Q(d_latch_7_q));  // open: NOT_Q
  D_Latch d_latch_8 (.EN(PHI2), .D(not_8_out), .Q(d_latch_8_q));  // open: NOT_Q
  nor nor_1 (nor_1_out, d_latch_1_q, _0_IR);
  nor nor_2 (nor_2_out, d_latch_2_q, _0_IR);
  nor nor_3 (nor_3_out, d_latch_3_q, _0_IR);
  nor nor_4 (nor_4_out, d_latch_4_q, _0_IR);
  nor nor_5 (nor_5_out, d_latch_5_q, _0_IR);
  nor nor_6 (nor_6_out, d_latch_6_q, _0_IR);
  nor nor_7 (nor_7_out, d_latch_7_q, _0_IR);
  nor nor_8 (nor_8_out, d_latch_8_q, _0_IR);
  not not_9 (not_9_out, nor_4_out);
  nor nor1 (nor1_out, nor_1_out, nor_3_out, not_9_out);
  nor nor2 (nor2_out, nor_2_out, nor_5_out, nor_8_out);
  not not_10 (not_10_out, nor_1_out);
  not not_11 (not_11_out, nor_4_out);
  nor nor3 (nor3_out, not_10_out, nor_3_out, not_11_out, nor_5_out);
  not not_12 (not_12_out, nor_8_out);
  nor nor4 (nor4_out, nor_1_out, nor_3_out, nor_4_out, nor_5_out, not_12_out);
  not not_13 (nPD0, nor_1_out);
  not not_14 (nPD1, nor_2_out);
  not not_15 (nPD2, nor_3_out);
  not not_16 (nPD3, nor_4_out);
  not not_17 (nPD4, nor_5_out);
  not not_18 (nPD5, nor_6_out);
  not not_19 (nPD6, nor_7_out);
  not not_20 (nPD7, nor_8_out);
  nand nand1 (nand1_out, nor1_out, not_21_out);
  not not_21 (not_21_out, nor2_out);
  nor nor5 (nor5_out, nor3_out, nor4_out);
  not not_22 (nIMPLIED, nor1_out);
  and and9 (nTWOCYCLE, nand1_out, nor5_out);
endmodule

module RANDOM_LOGIC (
  input  PHI1,
  input  X0,
  input  X1,
  input  X2,
  input  X3,
  input  X4,
  input  X5,
  input  X6,
  input  X7,
  input  X8,
  input  X9,
  input  X10,
  input  X11,
  input  X12,
  input  X13,
  input  X14,
  input  X15,
  input  X16,
  input  X17,
  input  X18,
  input  X19,
  input  X20,
  input  X21,
  input  X22,
  input  X23,
  input  X24,
  input  X25,
  input  X26,
  input  X27,
  input  X28,
  input  X29,
  input  X30,
  input  X31,
  input  X32,
  input  X33,
  input  X34,
  input  X35,
  input  X36,
  input  X37,
  input  X38,
  input  X39,
  input  X40,
  input  X41,
  input  X42,
  input  X43,
  input  X44,
  input  X45,
  input  X46,
  input  X47,
  input  X48,
  input  X49,
  input  X50,
  input  X51,
  input  X52,
  input  X53,
  input  X54,
  input  X55,
  input  X56,
  input  X57,
  input  X58,
  input  X59,
  input  X60,
  input  X61,
  input  X62,
  input  X63,
  input  X64,
  input  X65,
  input  X66,
  input  X67,
  input  X68,
  input  X69,
  input  X70,
  input  X71,
  input  X72,
  input  X73,
  input  X74,
  input  X75,
  input  X76,
  input  X77,
  input  X78,
  input  X79,
  input  X80,
  input  X81,
  input  X82,
  input  X83,
  input  X84,
  input  X85,
  input  X86,
  input  X87,
  input  X88,
  input  X89,
  input  X90,
  input  X91,
  input  X92,
  input  X93,
  input  X94,
  input  X95,
  input  X96,
  input  X97,
  input  X98,
  input  X99,
  input  X100,
  input  X101,
  input  X102,
  input  X103,
  input  X104,
  input  X105,
  input  X106,
  input  X107,
  input  X108,
  input  X109,
  input  X110,
  input  X111,
  input  X112,
  input  X113,
  input  X114,
  input  X115,
  input  X116,
  input  X117,
  input  X118,
  input  X119,
  input  X120,
  input  X121,
  input  X122,
  input  X123,
  input  X124,
  input  X125,
  input  X126,
  input  X127,
  input  X128,
  input  X129,
  input  PHI2,
  input  nIR5,
  input  nNMIP,
  input  RESP,
  input  nIRQP,
  input  AVR,
  input  ACR,
  input  SO,
  input  nTWOCYCLE,
  input  nIMPLIED,
  input  RDY,
  input  nPRDY,
  input  DB7,
  input  DB6,
  input  DB5,
  input  DB4,
  input  DB3,
  input  DB2,
  input  DB1,
  input  DB0,
  output FETCH,
  output nT0,
  output nT2,
  output nT3,
  output nT4,
  output nT5,
  output _0_ADL0,
  output _0_ADL1,
  output _0_ADL2,
  output Y_SB,
  output X_SB,
  output SB_Y,
  output SB_X,
  output S_SB,
  output S_ADL,
  output SB_S,
  output S_S,
  output nV_OUT,
  output nI_OUT,
  output nD_OUT,
  output nC_OUT,
  output nN_OUT,
  output nZ_OUT,
  output NDB_ADD,
  output DB_ADD,
  output _0_ADD,
  output SB_ADD,
  output ADL_ADD,
  output ANDS,
  output EORS,
  output ORS,
  output nACIN,
  output SUMS,
  output nDAA,
  output ADD_SB7,
  output ADD_SB06,
  output ADD_ADL,
  output nDSA,
  output SRS,
  output DL_ADL,
  output DL_DB,
  output DL_ADH,
  output ADH_ABH,
  output ADL_ABL,
  output SB_AC,
  output AC_SB,
  output _0_ADH0,
  output _0_ADH17,
  output AC_DB,
  output SB_DB,
  output SB_ADH,
  output ADL_PCL,
  output PCL_PCL,
  output PCH_ADH,
  output PCL_ADL,
  output PCH_DB,
  output PCL_DB,
  output ADH_PCH,
  output PCH_PCH,
  output TRESX,
  output _0_IR,
  output ENDS,
  output ENDX,
  output TRES1,
  output T1,
  output nT1X,
  output TRES2,
  output _1_PC,
  output P_DB,
  output IR5_I,
  output IR5_C,
  output IR5_D,
  output _0_V,
  output ACR_C,
  output DBZ_Z,
  output DB_N,
  output DB_P,
  output DB_C,
  output DB_V,
  output WR,
  output DB7_2,
  output DB6_2,
  output DB5_2,
  output DB4_2,
  output DB3_2,
  output DB2_2,
  output DB1_2,
  output DB0_2
);

  wire alu_setup_1_and, alu_setup_1_inc_sb, alu_setup_1_sr, BR0, BRANCH_LOGIC_brfw, BRANCH_LOGIC_nbrtaken,
       BRK6E, bus_control_1_pgx, bus_control_1_ztst, dispatch_1_acrl2, dispatch_1_stor,
       INTERRUPT_RESET_CONTROL_b_out, INTERRUPT_RESET_CONTROL_brk5_rdy, INTERRUPT_RESET_CONTROL_brk7,
       INTERRUPT_RESET_CONTROL_dores, INTERRUPT_RESET_CONTROL_ndonmi, nREADY, pc_setup_1_dl_pch,
       pc_setup_1_nadl_pcl, pc_setup_1_npch_pch, pc_setup_1_pc_db, regs_control_1_sbxy, regs_control_1_stkop,
       regs_control_1_stxy, T0, T5, T6;

  INT_RESET_CONTROL INTERRUPT_RESET_CONTROL (
    .PHI1(PHI1), .PHI2(PHI2), .nready(nREADY), .BRK5(X22), .nNMIP(nNMIP), .RESP(RESP), .BRK6E(BRK6E),
    .BRK7(INTERRUPT_RESET_CONTROL_brk7), .nDONMI(INTERRUPT_RESET_CONTROL_ndonmi),
    .DORES(INTERRUPT_RESET_CONTROL_dores), .B_OUT(INTERRUPT_RESET_CONTROL_b_out), .nIRQP(nIRQP),
    .nI_OUT(nI_OUT), .T0(T0), .BR2(X80), .BRK5_RDY(INTERRUPT_RESET_CONTROL_brk5_rdy));
  INT_VECTOR INTERRUPT_VECTOR (
    .PHI2(PHI2), .BRK5_RDY(INTERRUPT_RESET_CONTROL_brk5_rdy), .BRK7(INTERRUPT_RESET_CONTROL_brk7),
    .DORES(INTERRUPT_RESET_CONTROL_dores), .nDONMI(INTERRUPT_RESET_CONTROL_ndonmi), ._0_ADL0(_0_ADL0),
    ._0_ADL1(_0_ADL1), ._0_ADL2(_0_ADL2));
  REGS_CONTROL regs_control_1 (
    .nready(nREADY), .PHI1(PHI1), .STOR(dispatch_1_stor), .Y_SB(Y_SB), .X_SB(X_SB), .S_ADL(S_ADL),
    .SB_S(SB_S), .S_S(S_S), .STXY(regs_control_1_stxy), .SBXY(regs_control_1_sbxy),
    .STKOP(regs_control_1_stkop), .D0(X0), .D1(X1), .D2(X2), .D3(X3), .D4(X4), .D5(X5), .D6(X6), .D7(X7),
    .D8(X8), .D9(X9), .D10(X10), .D11(X11), .D12(X12), .D13(X13), .D14(X14), .D15(X15), .D16(X16), .D17(X17),
    .D18(X18), .D19(X19), .D20(X20), .D21(X21), .D22(X22), .D23(X23), .D24(X24), .D25(X25), .D26(X26),
    .D48(X48), .SB_X(SB_X), .SB_Y(SB_Y), .S_SB(S_SB), .D35(X35), .PHI2(PHI2));
  FLAGS flags_1 (
    .PHI1(PHI1), .PHI2(PHI2), .P_DB(P_DB), .B_OUT(INTERRUPT_RESET_CONTROL_b_out), .DB0(DB0), .DB1(DB1),
    .DB2(DB2), .DB3(DB3), .DB4(DB4), .DB5(DB5), .DB6(DB6), .DB7(DB7), .DB_P(DB_P), .DBZ_Z(DBZ_Z),
    .DB_N(DB_N), .IR5_C(IR5_C), .ACR_C(ACR_C), .DB_C(DB_C), .IR5_D(IR5_D), .IR5_I(IR5_I), .ACR(ACR),
    .nIR5(nIR5), .AVR(AVR), .D112(X112), .DB_V(DB_V), ._0_V(_0_V), .DB0_2(DB0_2), .DB1_2(DB1_2),
    .DB2_2(DB2_2), .DB3_2(DB3_2), .DB4_2(DB4_2), .DB5_2(DB5_2), .DB6_2(DB6_2), .DB7_2(DB7_2),
    .nZ_OUT(nZ_OUT), .nN_OUT(nN_OUT), .nC_OUT(nC_OUT), .nD_OUT(nD_OUT), .nI_OUT(nI_OUT), .nV_OUT(nV_OUT),
    .SO(SO), .BRK6E(BRK6E));
  ALU_SETUP alu_setup_1 (
    .NDB_ADD(NDB_ADD), .DB_ADD(DB_ADD), .D27(X27), ._0_ADD(_0_ADD), .D29(X29), .D30(X30), .SB_ADD(SB_ADD),
    .D31(X31), .D32(X32), .D33(X33), .ADL_ADD(ADL_ADD), .D34(X34), .D35(X35), .ANDS(ANDS), .D36(X36),
    .D37(X37), .D38(X38), .EORS(EORS), .D39(X39), .D40(X40), .ORS(ORS), .D41(X41), .D42(X42), .nACIN(nACIN),
    .D43(X43), .D44(X44), .D45(X45), .SRS(SRS), .D47(X47), .SUMS(SUMS), .D48(X48), .D49(X49), .nDAA(nDAA),
    .D50(X50), .D51(X51), .D52(X52), .ADD_SB7(ADD_SB7), .D53(X53), .D54(X54), .ADD_SB06(ADD_SB06), .D56(X56),
    .ADD_ADL(ADD_ADL), .nDSA(nDSA), .PHI1(PHI1), .PHI2(PHI2), .nready(nREADY), .T0(T0), .T5(T5),
    .STKOP(regs_control_1_stkop), .PGX(bus_control_1_pgx), .T1(T1), .T6(T6), .BRK6E(BRK6E), .BR3(X93),
    .nD_OUT(nD_OUT), .nC_OUT(nC_OUT), .D75(X75), .D76(X76), .D84(X84), .D85(X85), .D86(X86), .D87(X87),
    .D88(X88), .D89(X89), .INC_SB(alu_setup_1_inc_sb), .SR(alu_setup_1_sr), .D26(X26),
    .BRFW(BRANCH_LOGIC_brfw), .D69(X69), .D70(X70), .AND(alu_setup_1_and));
  and and_1 (BR0, X73, ~nPRDY);  // AND_Gate
  BUS_CONTROL bus_control_1 (
    .PHI1(PHI1), .PHI2(PHI2), .D58(X58), .D59(X59), .D60(X60), .D61(X61), .D62(X62), .D63(X63), .D64(X64),
    .D65(X65), .D66(X66), .D67(X67), .D68(X68), .D71(X71), .D72(X72), .D73(BR0), .D81(X81), .D82(X82),
    .D89(X89), .D90(X90), .D91(X91), .DL_ADH(DL_ADH), .DL_DB(DL_DB), .DL_ADL(DL_ADL), .BR2(X80),
    .SB_ADH(SB_ADH), .ADH_ABH(ADH_ABH), .ADL_ABL(ADL_ABL), .SB_AC(SB_AC), .AC_SB(AC_SB), .D57(X57),
    ._0_ADH17(_0_ADH17), .SB_DB(SB_DB), .BR3(X93), .nready(nREADY), .T2(X28), .PGX(bus_control_1_pgx),
    .D84(X84), .D129(X129), .D128(X128), .D101(X101), .D46(X46), .D48(X48), .D47(X47), .D45(X45),
    .INC_SB(alu_setup_1_inc_sb), .BRK6E(BRK6E), .D55(X55), .D83(X83), .STXY(regs_control_1_stxy),
    ._0_ADL0(_0_ADL0), .SBXY(regs_control_1_sbxy), .ZTST(bus_control_1_ztst), .DL_PCH(pc_setup_1_dl_pch),
    .ACRL2(dispatch_1_acrl2), .STOR(dispatch_1_stor), .nPCH_PCH(pc_setup_1_npch_pch), .T6(T6), .T5(T5),
    .T1(T1), .D56(X56), .T0(T0), .D74(X74), .D79(X79), .AC_DB(AC_DB), .AND(alu_setup_1_and), ._0_ADH0(_0_ADH0));
  PC_SETUP pc_setup_1 (
    .BR0(BR0), .PHI1(PHI1), .PHI2(PHI2), .D56(X56), .D77(X77), .D78(X78), .D83(X83), .D84(X84), .D94(X94),
    .D95(X95), .D96(X96), .D129(X129), .nready(nREADY), .BR3(X93), .BR2(X80), .T0(T0), .T1(T1),
    .PCL_DB(PCL_DB), .PCH_DB(PCH_DB), .PC_DB(pc_setup_1_pc_db), .PCL_ADL(PCL_ADL), .PCH_ADH(PCH_ADH),
    .PCL_PCL(PCL_PCL), .ADL_PCL(ADL_PCL), .DL_PCH(pc_setup_1_dl_pch), .nADL_PCL(pc_setup_1_nadl_pcl),
    .ADH_PCH(ADH_PCH), .PCH_PCH(PCH_PCH), .nPCH_PCH(pc_setup_1_npch_pch));
  DISPATCH dispatch_1 (
    .PHI1(PHI1), .PHI2(PHI2), .BRK6E(BRK6E), .BR2(X80), .RESP(RESP), .ACR(ACR), .D91(X91), .D92(X92),
    .D106(X106), .D107(X107), .D111(X111), .D122(X122), .D123(X123), .D124(X124), .D125(X125),
    .B_OUT(INTERRUPT_RESET_CONTROL_b_out), .nBRTAKEN(BRANCH_LOGIC_nbrtaken), .nTWOCYCLE(nTWOCYCLE),
    .RDY(RDY), .T5(T5), .T6(T6), .TRESX(TRESX), ._0_IR(_0_IR), .FETCH(FETCH), .ENDS_Debug(ENDS),
    .ENDX_Debug(ENDX), .TRES1(TRES1), .T0(T0), .nT1X(nT1X), .nready(nREADY), ._1_PC(_1_PC), .D97(X97),
    .D98(X98), .D100(X100), .BR3(X93), .D96(X96), .STOR(dispatch_1_stor),
    .DORES(INTERRUPT_RESET_CONTROL_dores), .D101(X101), .D102(X102), .D103(X103), .D104(X104), .D105(X105),
    .PC_DB(pc_setup_1_pc_db), .BRFW(BRANCH_LOGIC_brfw), .nIMPLIED(nIMPLIED), .nADL_PCL(pc_setup_1_nadl_pcl),
    .TRES2(TRES2), .T1(T1), .nT0(nT0), .ACRL2(dispatch_1_acrl2), .WR(WR));
  FLAGS_CONTROL flags_control_1 (
    .PHI2(PHI2), .D98(X98), .D99(X99), .D108(X108), .D110(X110), .D120(X120), .D127(X127), .D107(X107),
    .T6(T6), .D109(X109), .D112(X112), .D116(X116), .D117(X117), .D118(X118), .D119(X119), .D114(X114),
    .D115(X115), .nready(nREADY), .SR(alu_setup_1_sr), .D113(X113), .P_DB(P_DB), .IR5_I(IR5_I),
    .IR5_C(IR5_C), .IR5_D(IR5_D), ._0_V(_0_V), .ACR_C(ACR_C), .DBZ_Z(DBZ_Z), .DB_N(DB_N), .DB_P(DB_P),
    .DB_C(DB_C), .DB_V(DB_V), .ZTST(bus_control_1_ztst));
  BRANCH_LOGIC BRANCH_LOGIC (
    .nIR5(nIR5), .D126(X126), .nC_OUT(nC_OUT), .nV_OUT(nV_OUT), .nN_OUT(nN_OUT), .nZ_OUT(nZ_OUT),
    .PHI1(PHI1), .PHI2(PHI2), .DB7(DB7), .BR2(X80), .nBRTAKEN(BRANCH_LOGIC_nbrtaken),
    .BRFW(BRANCH_LOGIC_brfw), .D121(X121));
  EXTENDED_CYCLE_COUNTER extended_cycle_counter_1 (
    .T1(T1), .nT2(nT2), .nT3(nT3), .nT4(nT4), .PHI1(PHI1), .nready(nREADY), .TRES2(TRES2), .nT5(nT5),
    .PHI2(PHI2));

  // Other names for the same wires on the sheet: BR2 = X80; BR3 = X93; T2 = X28

  // Notes on the sheet:
  //   BRK5
  //   JSR2
  //   STK2
  //   Branch T0 Skip
  //   Push/pull
endmodule

module NMI_FF (
  input  nNMI,
  input  PHI2,
  output NMIP
);

  wire and_1_out, and_2_out, nor_1_out, nor_2_out, not_1_out;

  not not_1 (not_1_out, nNMI);
  and and_1 (and_1_out, not_1_out, PHI2);
  nor nor_1 (nor_1_out, and_2_out, nor_2_out);
  and and_2 (and_2_out, nNMI, PHI2);
  nor nor_2 (nor_2_out, nor_1_out, and_1_out);
  not not_2 (NMIP, nor_2_out);
endmodule

module INT_RESET_CONTROL (
  input  PHI1,
  input  PHI2,
  input  BRK5,
  input  nready,
  input  RESP,
  input  nNMIP,
  input  BR2,
  input  T0,
  input  nIRQP,
  input  nI_OUT,
  output BRK6E,
  output BRK7,
  output BRK5_RDY,
  output DORES,
  output nDONMI,
  output B_OUT
);

  wire and_2_out, and_3_out, b_latch1_q, b_latch2_q, brk5_latch_q, brk6_latch1_not_q, brk6_latch2_not_q,
       brk6e_latch_q, brk7_latch_not_q, delay_latch1_not_q, delay_latch2_q, donmi_latch_q, ff1_latch_q,
       ff2_latch_q, nand_1_out, nand_2_out, nand_3_out, nmip_latch_q, nor_1_out, nor_2_out, nor_3_out,
       nor_4_out, nor_5_out, nor_6_out, nor_9_out, not_1_out, not_2_out, not_3_out, not_4_out, or_1_out,
       or_2_out, res_latch1_q, res_latch2_q;

  and and_1 (BRK5_RDY, BRK5, not_1_out);
  not not_1 (not_1_out, nready);
  not not_2 (not_2_out, brk5_latch_q);
  D_Latch brk5_latch (.EN(PHI2), .D(BRK5_RDY), .Q(brk5_latch_q));  // open: NOT_Q
  D_Latch res_latch1 (.EN(PHI2), .D(RESP), .Q(res_latch1_q));  // open: NOT_Q
  D_Latch res_latch2 (.EN(PHI1), .D(nor_4_out), .Q(res_latch2_q));  // open: NOT_Q
  D_Latch brk7_latch (.EN(PHI2), .D(BRK7), .NOT_Q(brk7_latch_not_q));  // open: Q
  D_Latch nmip_latch (.EN(PHI1), .D(nNMIP), .Q(nmip_latch_q));  // open: NOT_Q
  D_Latch delay_latch1 (.EN(PHI2), .D(nDONMI), .NOT_Q(delay_latch1_not_q));  // open: Q
  D_Latch ff1_latch (.EN(PHI2), .D(nDONMI), .Q(ff1_latch_q));  // open: NOT_Q
  D_Latch brk6e_latch (.EN(PHI1), .D(BRK6E), .Q(brk6e_latch_q));  // open: NOT_Q
  or or_1 (or_1_out, nIRQP, not_3_out);
  not not_3 (not_3_out, nI_OUT);
  D_Latch b_latch2 (.EN(PHI1), .D(nor_9_out), .Q(b_latch2_q));  // open: NOT_Q
  not not_4 (not_4_out, b_latch2_q);
  and and_2 (and_2_out, not_2_out, nand_1_out);
  nand nand_1 (nand_1_out, nready, brk6_latch1_not_q);
  nor nor_1 (nor_1_out, res_latch1_q, res_latch2_q);
  nor nor_2 (nor_2_out, nmip_latch_q, nor_6_out);
  D_Latch ff2_latch (.EN(PHI2), .D(nor_2_out), .Q(ff2_latch_q));  // open: NOT_Q
  D_Latch delay_latch2 (.EN(PHI1), .D(delay_latch1_not_q), .Q(delay_latch2_q));  // open: NOT_Q
  nor nor_3 (nor_3_out, ff1_latch_q, brk6e_latch_q);
  nand nand_2 (nand_2_out, or_1_out, nDONMI);
  and and_3 (and_3_out, nand_3_out, not_4_out);
  D_Latch brk6_latch1 (.EN(PHI1), .D(and_2_out), .NOT_Q(brk6_latch1_not_q));  // open: Q
  nor nor_4 (nor_4_out, nor_1_out, BRK6E);
  nor nor_5 (nor_5_out, brk7_latch_not_q, nNMIP, nor_2_out);
  nor nor_6 (nor_6_out, ff2_latch_q, delay_latch2_q);
  nor nor_7 (nDONMI, donmi_latch_q, nor_3_out);
  or or_2 (or_2_out, BR2, T0);
  D_Latch b_latch1 (.EN(PHI2), .D(and_3_out), .Q(b_latch1_q));  // open: NOT_Q
  D_Latch brk6_latch2 (.EN(PHI2), .D(brk6_latch1_not_q), .NOT_Q(brk6_latch2_not_q));  // open: Q
  nor nor_8 (BRK7, brk6_latch1_not_q, BRK5_RDY);
  not not_5 (DORES, nor_1_out);
  D_Latch donmi_latch (.EN(PHI1), .D(nor_5_out), .Q(donmi_latch_q));  // open: NOT_Q
  nand nand_3 (nand_3_out, or_2_out, nand_2_out);
  nor nor_9 (nor_9_out, b_latch1_q, BRK6E);
  nor nor_10 (BRK6E, brk6_latch2_not_q, nready);
  nor nor_11 (B_OUT, DORES, nor_9_out);

  // Notes on the sheet:
  //   /NMIP
  //   /IRQP
  //   INTERRUPT CYCLE 6-7
  //   BRK_FF
  //   RESET FLIP/FLOP
  //   RES_FF
  //   NMI EDGE DETECT
  //   NMI_FF1
  //   INTERRUPT CHECK
  //   BR2
  //   T0
  //   B FLAG
  //   B_FF
  //   NMI_FF2
  //   /DONMI
  //   /DONMI
endmodule

module INT_VECTOR (
  input  PHI2,
  input  BRK5_RDY,
  input  BRK7,
  input  DORES,
  input  nDONMI,
  output _0_ADL0,
  output _0_ADL1,
  output _0_ADL2
);

  wire nor_1_out, nor_2_out, not_1_out, not_2_out, not_3_out, zadl2_latch_not_q;

  not not_1 (not_1_out, DORES);
  not not_2 (not_2_out, BRK5_RDY);
  nor nor_1 (nor_1_out, BRK7, not_1_out);
  not not_3 (not_3_out, nor_1_out);
  nor nor_2 (nor_2_out, BRK7, DORES, nDONMI);
  D_Latch zadl0_latch (.EN(PHI2), .D(not_2_out), .NOT_Q(_0_ADL0));  // open: Q
  D_Latch zadl1_latch (.EN(PHI2), .D(not_3_out), .NOT_Q(_0_ADL1));  // open: Q
  D_Latch zadl2_latch (.EN(PHI2), .D(nor_2_out), .NOT_Q(zadl2_latch_not_q));  // open: Q
  not not_4 (_0_ADL2, zadl2_latch_not_q);

  // Notes on the sheet:
  //   FFFA:NMI, 1010
  //   FFFC:RESET, 1100
  //   FFFE:IRQ/BRK, 1110
endmodule

module REGS_CONTROL (
  input  PHI1,
  input  PHI2,
  input  STOR,
  input  D0,
  input  D1,
  input  D2,
  input  D3,
  input  D4,
  input  D5,
  input  D6,
  input  D7,
  input  D8,
  input  D9,
  input  D10,
  input  D11,
  input  D12,
  input  D13,
  input  D14,
  input  D15,
  input  D16,
  input  D17,
  input  D18,
  input  D19,
  input  D20,
  input  D21,
  input  D22,
  input  D23,
  input  D24,
  input  D25,
  input  D26,
  input  D48,
  input  nready,
  input  D35,
  output Y_SB,
  output STXY,
  output X_SB,
  output S_SB,
  output SB_X,
  output SBXY,
  output SB_Y,
  output SB_S,
  output S_S,
  output STKOP,
  output S_ADL
);

  wire and_1_out, and_2_out, and_3_out, and_4_out, and_5_out, and_6_out, and_7_out, nor_1_out, nor_2_out,
       nor_3_out, nor_4_out, nor_5_out, nor_6_out, nor_8_out, nor_9_out, nor_11_out, nor_12_out, nor_13_out,
       nor_14_out, nor_15_out, nor_16_out, not_1_out, not_2_out, not_3_out, not_4_out, nready_latch_not_q,
       nready_latch_q, sadl_latch_not_q, sbs_latch_q, sbx_latch_q, sby_latch_q, ss_latch_q, ssb_latch_not_q,
       xsb_latch_q, ysb_latch_q;

  and and_1 (and_1_out, D6, D7);
  and and_2 (and_2_out, D6, not_1_out);
  not not_1 (not_1_out, D7);
  nor nor_1 (nor_1_out, D14, D15, D16);
  not not_2 (not_2_out, D17);
  nor nor_2 (nor_2_out, D18, D19, D20);
  not not_3 (not_3_out, D48);
  nor nor_3 (nor_3_out, D21, D22, D23, D24, D25, D26);
  and and_3 (and_3_out, STOR, D0);
  and and_4 (and_4_out, STOR, D12);
  D_Latch nready_latch (.EN(PHI1), .D(nready), .Q(nready_latch_q), .NOT_Q(nready_latch_not_q));
  nor nor_4 (nor_4_out, not_3_out, nready);
  nor nor_5 (nor_5_out, D1, D2, D3, D4, D5, and_1_out, and_3_out);
  nor nor_6 (nor_6_out, and_4_out, and_2_out, D8, D9, D10, D11, D13);
  and and_5 (and_5_out, D21, nready_latch_not_q);
  nor nor_7 (STKOP, nor_3_out, nready_latch_q);
  and and_6 (and_6_out, STOR, D0);
  and and_7 (and_7_out, STOR, D12);
  nand nand_1 (SBXY, nor_1_out, nor_2_out);
  nor nor_8 (nor_8_out, D13, nor_4_out, STKOP);
  nor nor_9 (nor_9_out, and_5_out, D35);
  not not_4 (not_4_out, nor_8_out);
  D_Latch ysb_latch (.EN(PHI2), .D(nor_5_out), .Q(ysb_latch_q));  // open: NOT_Q
  nor nor_10 (STXY, and_6_out, and_7_out);
  D_Latch xsb_latch (.EN(PHI2), .D(nor_6_out), .Q(xsb_latch_q));  // open: NOT_Q
  D_Latch ssb_latch (.EN(PHI2), .D(not_2_out), .NOT_Q(ssb_latch_not_q));  // open: Q
  D_Latch sbx_latch (.EN(PHI2), .D(nor_1_out), .Q(sbx_latch_q));  // open: NOT_Q
  D_Latch sby_latch (.EN(PHI2), .D(nor_2_out), .Q(sby_latch_q));  // open: NOT_Q
  D_Latch sbs_latch (.EN(PHI2), .D(nor_8_out), .Q(sbs_latch_q));  // open: NOT_Q
  D_Latch ss_latch (.EN(PHI2), .D(not_4_out), .Q(ss_latch_q));  // open: NOT_Q
  D_Latch sadl_latch (.EN(PHI2), .D(nor_9_out), .NOT_Q(sadl_latch_not_q));  // open: Q
  nor nor_11 (nor_11_out, ysb_latch_q, PHI2);
  buf buffer_1 (Y_SB, nor_11_out);
  buf buffer_2 (X_SB, nor_12_out);
  nor nor_12 (nor_12_out, xsb_latch_q, PHI2);
  buf buffer_3 (S_SB, ssb_latch_not_q);
  buf buffer_4 (SB_X, nor_13_out);
  nor nor_13 (nor_13_out, sbx_latch_q, PHI2);
  nor nor_14 (nor_14_out, sby_latch_q, PHI2);
  buf buffer_5 (SB_Y, nor_14_out);
  buf buffer_6 (SB_S, nor_15_out);
  nor nor_15 (nor_15_out, sbs_latch_q, PHI2);
  buf buffer_7 (S_S, nor_16_out);
  nor nor_16 (nor_16_out, ss_latch_q, PHI2);
  buf buffer_8 (S_ADL, sadl_latch_not_q);

  // Notes on the sheet:
  //   JSR2
  //   STK2
  //   TXS
  //   #SB/X
  //   #S/SB
  //   #SB/Y
  //   STOR
  //   STOR
  //   STKOP
  //   #Y/SB
  //   #X/SB
  //   #S/SB
  //   SBXY
  //   #SB/S
  //   #S/ADL
endmodule

module EXTENDED_CYCLE_COUNTER (
  input  PHI1,
  input  PHI2,
  input  TRES2,
  input  nready,
  input  T1,
  output nT2,
  output nT3,
  output nT4,
  output nT5
);

  wire multiplexer_1_out, multiplexer_2_out, multiplexer_3_out, multiplexer_4_out, nor_1_out, nor_2_out,
       nor_3_out, nor_4_out, t1_latch_not_q, t2_latch1_q, t2_latch2_not_q, t3_latch1_q, t3_latch2_not_q,
       t4_latch1_q, t4_latch2_not_q, t5_latch1_q, t5_latch2_not_q;

  D_Latch t1_latch (.EN(PHI2), .D(T1), .NOT_Q(t1_latch_not_q));  // open: Q
  Multiplexer #(.enable("false")) multiplexer_1 (
    .in0(t1_latch_not_q), .in1(t2_latch2_not_q), .out(multiplexer_1_out), .sel(nready));
  Multiplexer #(.enable("false")) multiplexer_2 (
    .in0(t2_latch2_not_q), .in1(t3_latch2_not_q), .out(multiplexer_2_out), .sel(nready));
  Multiplexer #(.enable("false")) multiplexer_3 (
    .in0(t3_latch2_not_q), .in1(t4_latch2_not_q), .out(multiplexer_3_out), .sel(nready));
  Multiplexer #(.enable("false")) multiplexer_4 (
    .in0(t4_latch2_not_q), .in1(t5_latch2_not_q), .out(multiplexer_4_out), .sel(nready));
  nor nor_1 (nor_1_out, TRES2, t2_latch1_q);
  nor nor_2 (nor_2_out, TRES2, t3_latch1_q);
  nor nor_3 (nor_3_out, TRES2, t4_latch1_q);
  nor nor_4 (nor_4_out, TRES2, t5_latch1_q);
  D_Latch t2_latch2 (.EN(PHI2), .D(nor_1_out), .NOT_Q(t2_latch2_not_q));  // open: Q
  D_Latch t2_latch1 (.EN(PHI1), .D(multiplexer_1_out), .Q(t2_latch1_q));  // open: NOT_Q
  D_Latch t3_latch2 (.EN(PHI2), .D(nor_2_out), .NOT_Q(t3_latch2_not_q));  // open: Q
  D_Latch t3_latch1 (.EN(PHI1), .D(multiplexer_2_out), .Q(t3_latch1_q));  // open: NOT_Q
  D_Latch t4_latch2 (.EN(PHI2), .D(nor_3_out), .NOT_Q(t4_latch2_not_q));  // open: Q
  D_Latch t4_latch1 (.EN(PHI1), .D(multiplexer_3_out), .Q(t4_latch1_q));  // open: NOT_Q
  D_Latch t5_latch2 (.EN(PHI2), .D(nor_4_out), .NOT_Q(t5_latch2_not_q));  // open: Q
  D_Latch t5_latch1 (.EN(PHI1), .D(multiplexer_4_out), .Q(t5_latch1_q));  // open: NOT_Q
  not not_1 (nT2, nor_1_out);
  not not_2 (nT3, nor_2_out);
  not not_3 (nT4, nor_3_out);
  not not_4 (nT5, nor_4_out);
endmodule
module ALU_SETUP (
  input  PHI1,
  input  PHI2,
  input  BRFW,
  input  nready,
  input  BRK6E,
  input  STKOP,
  input  D26,
  input  D27,
  input  D29,
  input  D30,
  input  D31,
  input  D32,
  input  D33,
  input  D34,
  input  D35,
  input  D36,
  input  D37,
  input  D38,
  input  D39,
  input  D40,
  input  D41,
  input  D42,
  input  D43,
  input  D44,
  input  D45,
  input  D47,
  input  D48,
  input  D49,
  input  D50,
  input  D51,
  input  D52,
  input  D53,
  input  D54,
  input  D56,
  input  D69,
  input  D70,
  input  D75,
  input  D76,
  input  D84,
  input  D85,
  input  D86,
  input  D87,
  input  D88,
  input  D89,
  input  T0,
  input  T1,
  input  T5,
  input  T6,
  input  PGX,
  input  BR3,
  input  nD_OUT,
  input  nC_OUT,
  output NDB_ADD,
  output DB_ADD,
  output _0_ADD,
  output SB_ADD,
  output ADL_ADD,
  output AND,
  output ANDS,
  output EORS,
  output ORS,
  output nACIN,
  output SRS,
  output SUMS,
  output nDAA,
  output ADD_SB7,
  output ADD_SB06,
  output ADD_ADL,
  output nDSA,
  output INC_SB,
  output SR
);

  wire acin_latch1_q, acin_latch2_q, acin_latch3_q, acin_latch4_q, acin_latch5_not_q, add_sb7_inst_nadd_sb7,
       addadl_latch_not_q, addsb06_latch_not_q, addsb7_latch_q, adladd_latch_q, and_1_out, and_2_out,
       and_3_out, ands_latch1_not_q, ands_latch2_not_q, daa_latch1_not_q, daa_latch2_not_q, dbadd_latch_q,
       dsa_latch1_not_q, eors_latch1_not_q, eors_latch2_not_q, nand_1_out, nand_2_out, nand_3_out,
       nand_4_out, nand_5_out, nand_6_out, ndbadd_latch_q, nor_1_out, nor_2_out, nor_3_out, nor_4_out,
       nor_5_out, nor_6_out, nor_7_out, nor_8_out, nor_9_out, nor_10_out, nor_11_out, nor_12_out, nor_13_out,
       nor_14_out, nor_15_out, nor_16_out, nor_17_out, nor_18_out, nor_19_out, nor_20_out, nor_21_out,
       nor_22_out, nor_23_out, not_1_out, not_2_out, not_4_out, not_5_out, not_6_out, not_9_out, not_10_out,
       not_11_out, not_12_out, not_13_out, not_14_out, not_15_out, or_1_out, or_2_out, ors_latch1_not_q,
       ors_latch2_not_q, sbadd_latch_q, srs_latch1_not_q, srs_latch2_not_q, sums_latch1_not_q,
       sums_latch2_not_q, zadd_latch_q;

  not not_1 (not_1_out, D34);
  not not_2 (not_2_out, nD_OUT);
  nor nor_1 (nor_1_out, D32, nready);
  and and_1 (and_1_out, D33, not_1_out);
  and and_2 (and_2_out, T5, D44);
  or or_1 (or_1_out, D52, D53);
  nor nor_2 (nor_2_out, D69, D70);
  not not_3 (AND, nor_2_out);
  and and_3 (and_3_out, D76, T5);
  not not_4 (not_4_out, D27);
  not not_5 (not_5_out, nor_1_out);
  nor nor_3 (nor_3_out, and_1_out, D35, D36, D37, D38, D39, nready);
  nor nor_4 (nor_4_out, D39, D40, D41, D42, D43, and_2_out);
  not not_6 (not_6_out, BR3);
  nor nor_5 (nor_5_out, D75, and_3_out);
  not not_7 (SR, nor_5_out);
  nor nor_6 (nor_6_out, D84, D85, D86, D87, D88, D89, D26);
  not not_8 (INC_SB, nor_4_out);
  nor nor_7 (nor_7_out, not_6_out, BRFW);
  nor nor_8 (nor_8_out, T0, T5);
  not not_9 (not_9_out, D47);
  nor nor_9 (nor_9_out, D49, D50, nor_7_out);
  not not_10 (not_10_out, nor_9_out);
  nor nor_10 (nor_10_out, nC_OUT, nor_8_out);
  nor nor_11 (nor_11_out, STKOP, D30, D31, D45, D48, INC_SB, D47, BRK6E, nready);
  nor nor_12 (nor_12_out, nor_3_out, not_9_out);
  nand nand_1 (nand_1_out, nor_10_out, or_1_out);
  not not_11 (not_11_out, D54);
  nand nand_2 (nand_2_out, nand_1_out, not_11_out);
  nand nand_3 (nand_3_out, D52, not_2_out);
  nor nor_13 (nor_13_out, nor_6_out, PGX);
  nor nor_14 (nor_14_out, nand_3_out, D51);
  nand nand_4 (nand_4_out, D51, not_2_out);
  or or_2 (or_2_out, not_10_out, D56, D51);
  D_Latch acin_latch1 (.EN(PHI2), .D(nor_12_out), .Q(acin_latch1_q));  // open: NOT_Q
  D_Latch acin_latch2 (.EN(PHI2), .D(INC_SB), .Q(acin_latch2_q));  // open: NOT_Q
  D_Latch acin_latch3 (.EN(PHI2), .D(not_10_out), .Q(acin_latch3_q));  // open: NOT_Q
  D_Latch acin_latch4 (.EN(PHI2), .D(nand_2_out), .Q(acin_latch4_q));  // open: NOT_Q
  not not_12 (not_12_out, nor_13_out);
  not not_13 (not_13_out, nor_14_out);
  not not_14 (not_14_out, nready);
  nor nor_15 (nor_15_out, acin_latch1_q, acin_latch2_q, acin_latch3_q, acin_latch4_q);
  nand nand_5 (nand_5_out, or_2_out, not_14_out);
  ADD_SB7 add_sb7_inst (
    .PHI1(PHI1), .PHI2(PHI2), .nC_OUT(nC_OUT), .nready(nready), .SR(SR), .nROR(not_4_out),
    .nADD_SB7(add_sb7_inst_nadd_sb7));
  nor nor_16 (nor_16_out, T6, STKOP, D56, T1, PGX);
  nand nand_6 (nand_6_out, nand_5_out, nor_3_out);
  nor nor_17 (nor_17_out, AND, D29, not_5_out, SR);
  nor nor_18 (nor_18_out, nor_16_out, add_sb7_inst_nadd_sb7);
  not not_15 (not_15_out, nor_11_out);
  D_Latch ndbadd_latch (.EN(PHI2), .D(nand_5_out), .Q(ndbadd_latch_q));  // open: NOT_Q
  D_Latch dbadd_latch (.EN(PHI2), .D(nand_6_out), .Q(dbadd_latch_q));  // open: NOT_Q
  D_Latch zadd_latch (.EN(PHI2), .D(nor_11_out), .Q(zadd_latch_q));  // open: NOT_Q
  D_Latch sbadd_latch (.EN(PHI2), .D(not_15_out), .Q(sbadd_latch_q));  // open: NOT_Q
  D_Latch adladd_latch (.EN(PHI2), .D(nor_3_out), .Q(adladd_latch_q));  // open: NOT_Q
  D_Latch ands_latch1 (.EN(PHI2), .D(AND), .NOT_Q(ands_latch1_not_q));  // open: Q
  D_Latch eors_latch1 (.EN(PHI2), .D(D29), .NOT_Q(eors_latch1_not_q));  // open: Q
  D_Latch ors_latch1 (.EN(PHI2), .D(not_5_out), .NOT_Q(ors_latch1_not_q));  // open: Q
  D_Latch srs_latch1 (.EN(PHI2), .D(SR), .NOT_Q(srs_latch1_not_q));  // open: Q
  D_Latch sums_latch1 (.EN(PHI2), .D(nor_17_out), .NOT_Q(sums_latch1_not_q));  // open: Q
  D_Latch daa_latch1 (.EN(PHI2), .D(not_13_out), .NOT_Q(daa_latch1_not_q));  // open: Q
  D_Latch addsb7_latch (.EN(PHI2), .D(nor_18_out), .Q(addsb7_latch_q));  // open: NOT_Q
  D_Latch addsb06_latch (.EN(PHI2), .D(nor_16_out), .NOT_Q(addsb06_latch_not_q));  // open: Q
  D_Latch addadl_latch (.EN(PHI2), .D(not_12_out), .NOT_Q(addadl_latch_not_q));  // open: Q
  D_Latch dsa_latch1 (.EN(PHI2), .D(nand_4_out), .NOT_Q(dsa_latch1_not_q));  // open: Q
  nor nor_19 (nor_19_out, ndbadd_latch_q, PHI2);
  nor nor_20 (nor_20_out, dbadd_latch_q, PHI2);
  nor nor_21 (nor_21_out, zadd_latch_q, PHI2);
  nor nor_22 (nor_22_out, sbadd_latch_q, PHI2);
  nor nor_23 (nor_23_out, adladd_latch_q, PHI2);
  D_Latch ands_latch2 (.EN(PHI1), .D(ands_latch1_not_q), .NOT_Q(ands_latch2_not_q));  // open: Q
  buf buffer_1 (ANDS, ands_latch2_not_q);
  D_Latch eors_latch2 (.EN(PHI1), .D(eors_latch1_not_q), .NOT_Q(eors_latch2_not_q));  // open: Q
  buf buffer_2 (EORS, eors_latch2_not_q);
  D_Latch ors_latch2 (.EN(PHI1), .D(ors_latch1_not_q), .NOT_Q(ors_latch2_not_q));  // open: Q
  buf buffer_3 (ORS, ors_latch2_not_q);
  D_Latch acin_latch5 (.EN(PHI1), .D(nor_15_out), .NOT_Q(acin_latch5_not_q));  // open: Q
  not not_16 (nACIN, acin_latch5_not_q);
  D_Latch srs_latch2 (.EN(PHI1), .D(srs_latch1_not_q), .NOT_Q(srs_latch2_not_q));  // open: Q
  buf buffer_4 (SRS, srs_latch2_not_q);
  D_Latch sums_latch2 (.EN(PHI1), .D(sums_latch1_not_q), .NOT_Q(sums_latch2_not_q));  // open: Q
  buf buffer_5 (SUMS, sums_latch2_not_q);
  D_Latch daa_latch2 (.EN(PHI1), .D(daa_latch1_not_q), .NOT_Q(daa_latch2_not_q));  // open: Q
  buf buffer_6 (nDAA, daa_latch2_not_q);
  buf buffer_7 (ADD_SB7, addsb7_latch_q);
  buf buffer_8 (ADD_SB06, addsb06_latch_not_q);
  buf buffer_9 (ADD_ADL, addadl_latch_not_q);
  D_Latch dsa_latch2 (.EN(PHI1), .D(dsa_latch1_not_q), .NOT_Q(nDSA));  // open: Q
  buf buffer_10 (NDB_ADD, nor_19_out);
  buf buffer_11 (DB_ADD, nor_20_out);
  buf buffer_12 (_0_ADD, nor_21_out);
  buf buffer_13 (SB_ADD, nor_22_out);
  buf buffer_14 (ADL_ADD, nor_23_out);

  // Other names for the same wires on the sheet: JSR_5 = D56; RTI_5 = D26; RTS_5 = D84; SBC0 = D51

  // Notes on the sheet:
  //   ROR
  //   EOR
  //   STK2
  //   RET
  //   JSR2
  //   D_OUT
  //   OR
  //   NOADL
  //   #ADL/ADD
  //   BRX
  //   SB/ADD
  //   CSET
  //   PGX
  //   /ACIN
  //   #NDB/ADD
  //   #ADD/SB7
  //   #ADD/SB06
  //   #ADL/ADD
  //   care!
endmodule

module BRANCH_LOGIC (
  input  nIR5,
  input  D121,
  input  D126,
  input  nC_OUT,
  input  nV_OUT,
  input  nN_OUT,
  input  nZ_OUT,
  input  PHI1,
  input  PHI2,
  input  DB7,
  input  BR2,
  output nBRTAKEN,
  output BRFW
);

  wire br2_latch_q, brfw_latch1_not_q, brfw_latch2_q, multiplexer_1_out, nor_1_out, nor_2_out, nor_3_out,
       nor_4_out, nor_5_out, not_1_out, not_2_out, not_3_out, not_4_out, not_5_out, not_6_out;

  not not_1 (not_1_out, D121);
  not not_2 (not_2_out, D126);
  not not_3 (not_3_out, D126);
  not not_4 (not_4_out, D121);
  not not_5 (not_5_out, DB7);
  D_Latch br2_latch (.EN(PHI2), .D(BR2), .Q(br2_latch_q));  // open: NOT_Q
  D_Latch brfw_latch2 (.EN(PHI2), .D(brfw_latch1_not_q), .Q(brfw_latch2_q));  // open: NOT_Q
  nor nor_1 (nor_1_out, nC_OUT, D126, not_1_out);
  nor nor_2 (nor_2_out, nV_OUT, D121, not_2_out);
  nor nor_3 (nor_3_out, nN_OUT, not_3_out, not_4_out);
  nor nor_4 (nor_4_out, D126, D121, nZ_OUT);
  nor nor_5 (nor_5_out, nor_1_out, nor_2_out, nor_3_out, nor_4_out);
  Multiplexer #(.enable("false")) multiplexer_1 (
    .in0(brfw_latch2_q), .in1(not_5_out), .out(multiplexer_1_out), .sel(br2_latch_q));
  xor xor_1 (nBRTAKEN, nIR5, nor_5_out);
  not not_6 (not_6_out, multiplexer_1_out);
  D_Latch brfw_latch1 (.EN(PHI1), .D(not_6_out), .NOT_Q(brfw_latch1_not_q));  // open: Q
  not not_7 (BRFW, brfw_latch1_not_q);

  // Notes on the sheet:
  //   /IR6
  //   /IR7
  //   2-MUX
  //   BRFW_FF
endmodule

// PROGRAM COUNTER SETUP
module PC_SETUP (
  input  PHI1,
  input  PHI2,
  input  D56,
  input  D77,
  input  D78,
  input  D83,
  input  D84,
  input  D94,
  input  D95,
  input  D96,
  input  D129,
  input  nready,
  input  BR3,
  input  BR2,
  input  T0,
  input  T1,
  input  BR0,
  output PCL_DB,
  output PCH_DB,
  output PC_DB,
  output PCL_ADL,
  output PCH_ADH,
  output PCL_PCL,
  output ADL_PCL,
  output nADL_PCL,
  output DL_PCH,
  output ADH_PCH,
  output PCH_PCH,
  output nPCH_PCH
);

  wire adh_pch_latch_q, adl_pcl_latch_q, and_1_out, and_2_out, nor_1_out, nor_2_out, nor_3_out, nor_4_out,
       nor_5_out, nor_8_out, nor_9_out, nor_10_out, nor_11_out, nor_12_out, nor_13_out, nor_14_out,
       nor_15_out, not_1_out, not_2_out, not_3_out, not_5_out, nready_latch_q, pch_adh_latch_not_q,
       pch_db_latch1_q, pch_db_latch2_not_q, pch_pch_latch_q, pcl_adl_latch_not_q, pcl_db_latch1_not_q,
       pcl_db_latch2_not_q, pcl_pcl_latch_q;

  nor nor_1 (nor_1_out, D77, D78);
  and and_1 (and_1_out, D83, ~D129);  // AND_Gate
  nor nor_2 (nor_2_out, D94, D95, D96);
  D_Latch pch_db_latch1 (.EN(PHI2), .D(nor_1_out), .Q(pch_db_latch1_q));  // open: NOT_Q
  D_Latch nready_latch (.EN(PHI1), .D(nready), .Q(nready_latch_q));  // open: NOT_Q
  nor nor_3 (nor_3_out, pch_db_latch1_q, nready);
  nor nor_4 (nor_4_out, nor_2_out, nready_latch_q);
  not not_1 (not_1_out, nready_latch_q);
  not not_2 (not_2_out, T0);
  nor nor_5 (nor_5_out, nor_4_out, not_2_out);
  not not_3 (not_3_out, nor_8_out);
  and and_2 (and_2_out, not_1_out, BR3);
  nor nor_6 (DL_PCH, not_2_out, nor_2_out);
  D_Latch pcl_db_latch1 (.EN(PHI1), .D(nor_3_out), .NOT_Q(pcl_db_latch1_not_q));  // open: Q
  nor nor_7 (nADL_PCL, not_3_out, D84, T0, and_2_out);
  nand nand_1 (PC_DB, pcl_db_latch1_not_q, nor_1_out);
  nor nor_8 (nor_8_out, T1, D56, and_1_out, nor_5_out, BR2);
  nor nor_9 (nor_9_out, D84, and_1_out, T0, T1, BR2, BR3);
  nor nor_10 (nor_10_out, nor_8_out, DL_PCH, BR0);
  not not_4 (nPCH_PCH, nor_9_out);
  nor nor_11 (nor_11_out, nor_10_out, BR3);
  not not_5 (not_5_out, nADL_PCL);
  D_Latch pcl_db_latch2 (.EN(PHI2), .D(pcl_db_latch1_not_q), .NOT_Q(pcl_db_latch2_not_q));  // open: Q
  D_Latch pch_db_latch2 (.EN(PHI2), .D(nor_1_out), .NOT_Q(pch_db_latch2_not_q));  // open: Q
  D_Latch pcl_adl_latch (.EN(PHI2), .D(nor_8_out), .NOT_Q(pcl_adl_latch_not_q));  // open: Q
  D_Latch pch_adh_latch (.EN(PHI2), .D(nor_11_out), .NOT_Q(pch_adh_latch_not_q));  // open: Q
  D_Latch pcl_pcl_latch (.EN(PHI2), .D(not_5_out), .Q(pcl_pcl_latch_q));  // open: NOT_Q
  D_Latch adl_pcl_latch (.EN(PHI2), .D(nADL_PCL), .Q(adl_pcl_latch_q));  // open: NOT_Q
  D_Latch adh_pch_latch (.EN(PHI2), .D(nor_9_out), .Q(adh_pch_latch_q));  // open: NOT_Q
  D_Latch pch_pch_latch (.EN(PHI2), .D(nPCH_PCH), .Q(pch_pch_latch_q));  // open: NOT_Q
  nor nor_12 (nor_12_out, pcl_pcl_latch_q, PHI2);
  nor nor_13 (nor_13_out, adl_pcl_latch_q, PHI2);
  nor nor_14 (nor_14_out, adh_pch_latch_q, PHI2);
  nor nor_15 (nor_15_out, pch_pch_latch_q, PHI2);
  buf buffer_1 (PCL_DB, pcl_db_latch2_not_q);
  buf buffer_2 (PCH_DB, pch_db_latch2_not_q);
  buf buffer_3 (PCL_ADL, pcl_adl_latch_not_q);
  buf buffer_4 (PCH_ADH, pch_adh_latch_not_q);
  buf buffer_5 (PCL_PCL, nor_12_out);
  buf buffer_6 (ADL_PCL, nor_13_out);
  buf buffer_7 (ADH_PCH, nor_14_out);
  buf buffer_8 (PCH_PCH, nor_15_out);

  // Other names for the same wires on the sheet: RTS_5 = D84

  // Notes on the sheet:
  //   JSR/5
  //   Push/pull
  //   JB
  //   #PCH/DB
  //   ABS/2
  //   DL/PCH
  //   #PCL/DB
  //   PC/DB
  //   DL/PCH
  //   #PCL/ADL
  //   #ADL/PCL
  //   #ADH/PCH
endmodule

module DISPATCH (
  input  PHI1,
  input  PHI2,
  input  BRK6E,
  input  BR2,
  input  RESP,
  input  ACR,
  input  DORES,
  input  PC_DB,
  input  D91,
  input  D92,
  input  BR3,
  input  D96,
  input  D97,
  input  D98,
  input  D100,
  input  D101,
  input  D102,
  input  D103,
  input  D104,
  input  D105,
  input  D106,
  input  D107,
  input  D111,
  input  D122,
  input  D123,
  input  D124,
  input  D125,
  input  RDY,
  input  B_OUT,
  input  BRFW,
  input  nBRTAKEN,
  input  nTWOCYCLE,
  input  nADL_PCL,
  input  nIMPLIED,
  output ACRL2,
  output T5,
  output T6,
  output TRES2,
  output TRESX,
  output STOR,
  output ENDX_Debug,
  output ENDS_Debug,
  output _0_IR,
  output FETCH,
  output nready,
  output WR,
  output T1,
  output TRES1,
  output nT0,
  output T0,
  output nT1X,
  output _1_PC
);

  wire acr_latch1_not_q, and_1_out, and_2_out, and_3_out, and_4_out, and_5_out, and_6_out, br_latch1_q,
       br_latch2_not_q, comp_latch1_q, comp_latch2_q, comp_latch3_q, ends_latch1_q, ends_latch2_q,
       fetch_latch_not_q, ipc_latch1_q, ipc_latch2_q, ipc_latch3_q, multiplexer_1_out, nand_1_out,
       nand_2_out, nMemOP, nor_1_out, nor_4_out, nor_5_out, nor_6_out, nor_7_out, nor_8_out, nor_9_out,
       nor_10_out, nor_11_out, nor_12_out, nor_13_out, nor_16_out, nor_17_out, nor_18_out, nor_19_out,
       nor_20_out, nor_21_out, nor_23_out, nor_24_out, nor_25_out, nor_26_out, nor_28_out, nor_29_out,
       nor_30_out, nor_32_out, not_1_out, not_2_out, not_3_out, not_4_out, not_5_out, not_6_out, not_7_out,
       not_8_out, not_9_out, not_10_out, not_11_out, not_12_out, NotReadyPhi1, nready_latch_q, nSHIFT,
       or_1_out, rdydelay_latch1_not_q, ready_latch1_not_q, ready_latch2_q, step_latch1_q, step_latch2_q,
       t0_latch_q, t1x_latch_q, t5_latch2_q, t6_latch1_not_q, t6_latch2_not_q, t56_latch_q, tresx_latch1_q,
       tresx_latch2_not_q, wr_latch_q, xor_1_out;

  nor nor_1 (nor_1_out, D91, D92);
  not not_1 (not_1_out, D97);
  nor nor_2 (nSHIFT, D106, D107);
  nor nor_3 (nMemOP, D111, D122, D123, D124, D125);
  nor nor_4 (nor_4_out, BR2, BR3);
  not not_2 (not_2_out, ACR);
  not not_3 (not_3_out, NotReadyPhi1);
  nor nor_5 (nor_5_out, D100, D101, D102, D103, D104, D105);
  not not_4 (not_4_out, nor_5_out);
  not not_5 (not_5_out, nor_4_out);
  not not_6 (not_6_out, nIMPLIED);
  and and_1 (and_1_out, not_2_out, not_3_out);
  nor nor_6 (nor_6_out, not_3_out, ACRL2);
  and and_2 (and_2_out, nBRTAKEN, BR2);
  not not_7 (not_7_out, BR3);
  and and_3 (and_3_out, nBRTAKEN, BR2);
  nor nor_7 (nor_7_out, nADL_PCL, not_5_out);
  nor nor_8 (nor_8_out, and_1_out, nor_6_out);
  nor nor_9 (nor_9_out, STOR, PC_DB, D98, D100, T6, T5);
  nor nor_10 (nor_10_out, T0, and_2_out);
  Multiplexer #(.enable("false")) multiplexer_1 (
    .in0(nor_10_out), .in1(not_8_out), .out(multiplexer_1_out), .sel(nready));
  not not_8 (not_8_out, T1);
  nor nor_11 (nor_11_out, not_7_out, NotReadyPhi1);
  D_Latch rdydelay_latch1 (.EN(PHI1), .D(nready), .NOT_Q(rdydelay_latch1_not_q));  // open: Q
  nor nor_12 (nor_12_out, and_3_out, nor_7_out);
  D_Latch acr_latch1 (.EN(PHI1), .D(nor_8_out), .NOT_Q(acr_latch1_not_q));  // open: Q
  D_Latch acr_latch2 (.EN(PHI2), .D(acr_latch1_not_q), .NOT_Q(ACRL2));  // open: Q
  D_Latch tresx_latch1 (.EN(PHI2), .D(nor_1_out), .Q(tresx_latch1_q));  // open: NOT_Q
  not not_9 (not_9_out, nSHIFT);
  D_Latch wr_latch (.EN(PHI2), .D(nor_9_out), .Q(wr_latch_q));  // open: NOT_Q
  D_Latch ends_latch1 (.EN(PHI2), .D(multiplexer_1_out), .Q(ends_latch1_q));  // open: NOT_Q
  D_Latch ends_latch2 (.EN(PHI2), .D(RESP), .Q(ends_latch2_q));  // open: NOT_Q
  D_Latch nready_latch (.EN(PHI1), .D(not_10_out), .Q(nready_latch_q));  // open: NOT_Q
  not not_10 (not_10_out, nready);
  D_Latch br_latch2 (.EN(PHI2), .D(nor_11_out), .NOT_Q(br_latch2_not_q));  // open: Q
  xor xor_1 (xor_1_out, BRFW, not_11_out);
  not not_11 (not_11_out, ACR);
  D_Latch rdydelay_latch2 (.EN(PHI2), .D(rdydelay_latch1_not_q), .NOT_Q(NotReadyPhi1));  // open: Q
  D_Latch comp_latch1 (.EN(PHI1), .D(TRES1), .Q(comp_latch1_q));  // open: NOT_Q
  D_Latch comp_latch2 (.EN(PHI1), .D(nTWOCYCLE), .Q(comp_latch2_q));  // open: NOT_Q
  D_Latch comp_latch3 (.EN(PHI1), .D(TRESX), .Q(comp_latch3_q));  // open: NOT_Q
  D_Latch br_latch1 (.EN(PHI2), .D(nor_12_out), .Q(br_latch1_q));  // open: NOT_Q
  nand nand_1 (nand_1_out, nSHIFT, not_1_out);
  nor nor_13 (nor_13_out, D96, not_9_out, nMemOP);
  and and_4 (and_4_out, comp_latch2_q, comp_latch3_q);
  nor nor_14 (ENDX_Debug, nor_13_out, T6, not_4_out, BR3);
  nor nor_15 (ENDS_Debug, ends_latch1_q, ends_latch2_q);
  and and_5 (and_5_out, ~br_latch2_not_q, xor_1_out);  // AND_Gate
  nor nor_16 (nor_16_out, nSHIFT, nMemOP, nready);
  not not_12 (not_12_out, nready);
  nor nor_17 (nor_17_out, nor_8_out, tresx_latch1_q, nready, nand_1_out);
  nor nor_18 (nor_18_out, comp_latch1_q, and_4_out);
  nor nor_19 (nor_19_out, t0_latch_q, t1x_latch_q);
  and and_6 (and_6_out, t5_latch2_q, nready);
  D_Latch t56_latch (.EN(PHI2), .D(nor_16_out), .Q(t56_latch_q));  // open: NOT_Q
  nand nand_2 (nand_2_out, T5, not_12_out);
  nor nor_20 (nor_20_out, nready, ENDX_Debug);
  nor nor_21 (nor_21_out, RDY, ready_latch2_q);
  nor nor_22 (WR, nready, wr_latch_q, DORES);
  nor nor_23 (nor_23_out, nready_latch_q, RESP, step_latch2_q);
  nor nor_24 (nor_24_out, step_latch1_q, and_5_out);
  nor nor_25 (nor_25_out, nor_24_out, nready);
  nor nor_26 (nor_26_out, nor_25_out, ENDS_Debug);
  nor nor_27 (nT0, nor_18_out, nor_19_out);
  nor nor_28 (nor_28_out, t0_latch_q, nready);
  nor nor_29 (nor_29_out, nready, br_latch1_q, not_6_out);
  nor nor_30 (nor_30_out, and_6_out, t56_latch_q);
  D_Latch t6_latch1 (.EN(PHI2), .D(nand_2_out), .NOT_Q(t6_latch1_not_q));  // open: Q
  nor nor_31 (TRESX, nor_17_out, BRK6E, tresx_latch2_not_q);
  nor nor_32 (nor_32_out, RESP, ENDS_Debug, nor_20_out);
  D_Latch fetch_latch (.EN(PHI2), .D(T1), .NOT_Q(fetch_latch_not_q));  // open: Q
  D_Latch ready_latch1 (.EN(PHI2), .D(nor_21_out), .NOT_Q(ready_latch1_not_q));  // open: Q
  D_Latch ready_latch2 (.EN(PHI1), .D(WR), .Q(ready_latch2_q));  // open: NOT_Q
  D_Latch step_latch1 (.EN(PHI2), .D(nor_23_out), .Q(step_latch1_q));  // open: NOT_Q
  D_Latch step_latch2 (.EN(PHI1), .D(nor_24_out), .Q(step_latch2_q));  // open: NOT_Q
  D_Latch t1_latch (.EN(PHI1), .D(nor_26_out), .NOT_Q(T1));  // open: Q
  not not_13 (TRES1, nor_26_out);
  D_Latch t0_latch (.EN(PHI2), .D(nT0), .Q(t0_latch_q));  // open: NOT_Q
  D_Latch t1x_latch (.EN(PHI1), .D(nor_28_out), .Q(t1x_latch_q), .NOT_Q(nT1X));
  D_Latch ipc_latch1 (.EN(PHI1), .D(B_OUT), .Q(ipc_latch1_q));  // open: NOT_Q
  D_Latch ipc_latch2 (.EN(PHI1), .D(and_5_out), .Q(ipc_latch2_q));  // open: NOT_Q
  D_Latch ipc_latch3 (.EN(PHI1), .D(nor_29_out), .Q(ipc_latch3_q));  // open: NOT_Q
  D_Latch t5_latch2 (.EN(PHI2), .D(T5), .Q(t5_latch2_q));  // open: NOT_Q
  D_Latch t5_latch1 (.EN(PHI1), .D(nor_30_out), .NOT_Q(T5));  // open: Q
  D_Latch t6_latch2 (.EN(PHI1), .D(t6_latch1_not_q), .NOT_Q(t6_latch2_not_q));  // open: Q
  D_Latch tres2_latch (.EN(PHI1), .D(TRESX), .NOT_Q(TRES2));  // open: Q
  nor nor_33 (STOR, nMemOP, not_1_out);
  D_Latch tresx_latch2 (.EN(PHI2), .D(nor_32_out), .NOT_Q(tresx_latch2_not_q));  // open: Q
  not not_14 (nready, ready_latch1_not_q);
  or or_1 (or_1_out, ipc_latch2_q, ipc_latch3_q);
  not not_15 (T6, t6_latch2_not_q);
  nand nand_3 (_0_IR, B_OUT, FETCH);
  nor nor_34 (FETCH, fetch_latch_not_q, nready);
  not not_16 (T0, nT0);
  nand nand_4 (_1_PC, ipc_latch1_q, or_1_out);

  // Notes on the sheet:
  //   /STORE
  //   ACRL_FF
  //   STOR
  //   ReadyDelay
  //   TRES1
  //   ACRL1
  //   REST
  //   ENDS
  //   ENDS
  //   RDY
  //   STEP_FF
  //   ENDS
  //   WR
  //   T0_FF
  //   T5_FF
  //   RDY_FF
endmodule

// BUS CONTROL
module BUS_CONTROL (
  input  PHI1,
  input  PHI2,
  input  SBXY,
  input  D55,
  input  D57,
  input  D58,
  input  D59,
  input  D60,
  input  D61,
  input  D62,
  input  D63,
  input  D64,
  input  D65,
  input  D66,
  input  D67,
  input  D68,
  input  AND,
  input  D71,
  input  D72,
  input  D73,
  input  D74,
  input  D79,
  input  STOR,
  input  D81,
  input  D82,
  input  D84,
  input  D89,
  input  D90,
  input  D91,
  input  D83,
  input  D128,
  input  D129,
  input  _0_ADL0,
  input  BR2,
  input  ACRL2,
  input  DL_PCH,
  input  BR3,
  input  nready,
  input  T2,
  input  INC_SB,
  input  D45,
  input  BRK6E,
  input  D46,
  input  D47,
  input  D48,
  input  STXY,
  input  D101,
  input  nPCH_PCH,
  input  T0,
  input  T1,
  input  T5,
  input  T6,
  input  D56,
  output _0_ADH0,
  output _0_ADH17,
  output SB_AC,
  output ZTST,
  output ADL_ABL,
  output AC_SB,
  output SB_DB,
  output AC_DB,
  output PGX,
  output SB_ADH,
  output DL_ADH,
  output DL_ADL,
  output ADH_ABH,
  output DL_DB
);

  wire ac_db_latch_q, ac_sb_latch_q, adh_abh_latch_not_q, adl_abl_latch_not_q, and_1_out, and_2_out,
       and_3_out, and_4_out, and_5_out, and_6_out, dl_adh_latch_not_q, dl_adl_latch_not_q, dl_db_latch_not_q,
       nand_2_out, nand_3_out, nand_4_out, nand_5_out, nor_1_out, nor_2_out, nor_3_out, nor_4_out, nor_5_out,
       nor_6_out, nor_7_out, nor_8_out, nor_9_out, nor_10_out, nor_11_out, nor_12_out, nor_13_out,
       nor_14_out, nor_15_out, nor_16_out, nor_17_out, nor_18_out, nor_19_out, nor_20_out, nor_21_out,
       nor_22_out, nor_23_out, nor_24_out, nor_25_out, not_1_out, not_2_out, not_3_out, not_4_out, not_5_out,
       not_6_out, not_7_out, not_8_out, not_9_out, nready_latch_not_q, or_1_out, sb_ac_latch_q,
       sb_adh_latch_not_q, sb_db_latch_not_q, z_adh17_latch_not_q;

  not not_1 (not_1_out, D64);
  nor nor_1 (nor_1_out, D71, D72);
  not not_2 (not_2_out, D73);
  and and_1 (and_1_out, D79, STOR);
  nor nor_2 (nor_2_out, D81, D82);
  and and_2 (and_2_out, D90, ~D129);  // AND_Gate
  and and_3 (and_3_out, D83, ~D129);  // AND_Gate
  and and_4 (and_4_out, D128, ~D129);  // AND_Gate
  not not_3 (not_3_out, D48);
  nor nor_3 (nor_3_out, D58, D59, D60, D61, D62, D63, D64);
  and and_5 (and_5_out, not_1_out, D65);
  not not_4 (not_4_out, nor_1_out);
  nand nand_1 (PGX, nor_1_out, not_2_out);
  nor nor_4 (nor_4_out, D74, and_1_out);
  nor nor_5 (nor_5_out, D89, and_2_out, D91, D84);
  nor nor_6 (nor_6_out, and_3_out, T0);
  D_Latch nready_latch (.EN(PHI1), .D(nready), .NOT_Q(nready_latch_not_q));  // open: Q
  nor nor_7 (nor_7_out, INC_SB, D45, BRK6E, D46, D47, D48);
  nand nand_2 (nand_2_out, not_3_out, STXY);
  not not_5 (not_5_out, nor_3_out);
  nor nor_8 (nor_8_out, and_5_out, D66, D67, D68, AND);
  not not_6 (not_6_out, nor_5_out);
  nor nor_9 (nor_9_out, nor_6_out, and_4_out);
  nand nand_3 (nand_3_out, ACRL2, nready_latch_not_q);
  not not_7 (not_7_out, nor_7_out);
  nand nand_4 (nand_4_out, T5, D55);
  nor nor_10 (nor_10_out, SBXY, not_5_out, T6, AND);
  nor nor_11 (nor_11_out, not_4_out, nready);
  nor nor_12 (nor_12_out, PGX, BR3);
  nor nor_13 (nor_13_out, not_6_out, T2, nPCH_PCH, D56);
  not not_8 (not_8_out, nand_4_out);
  not not_9 (not_9_out, nor_2_out);
  nor nor_14 (nor_14_out, nor_10_out, AND);
  nor nor_15 (nor_15_out, nor_12_out, nand_3_out);
  nor nor_16 (nor_16_out, nready, nor_13_out);
  nor nor_17 (nor_17_out, D57, not_9_out);
  or or_1 (or_1_out, nor_15_out, nor_16_out);
  nor nor_18 (nor_18_out, T6, T5);
  nor nor_19 (nor_19_out, not_8_out, nor_14_out, D67, T1, BR2, nand_2_out);
  and and_6 (and_6_out, or_1_out, ~BR3);  // AND_Gate
  nand nand_5 (nand_5_out, nor_18_out, nor_11_out);
  nor nor_20 (nor_20_out, DL_PCH, not_6_out);
  nor nor_21 (nor_21_out, _0_ADL0, and_6_out);
  nor nor_22 (nor_22_out, BR2, nor_9_out, not_7_out, D101, T5);
  D_Latch z_adh0_latch (.EN(PHI2), .D(nor_2_out), .NOT_Q(_0_ADH0));  // open: Q
  D_Latch z_adh17_latch (.EN(PHI2), .D(nor_17_out), .NOT_Q(z_adh17_latch_not_q));  // open: Q
  D_Latch sb_ac_latch (.EN(PHI2), .D(nor_3_out), .Q(sb_ac_latch_q));  // open: NOT_Q
  D_Latch adl_abl_latch (.EN(PHI2), .D(nand_5_out), .NOT_Q(adl_abl_latch_not_q));  // open: Q
  D_Latch ac_sb_latch (.EN(PHI2), .D(nor_8_out), .Q(ac_sb_latch_q));  // open: NOT_Q
  D_Latch sb_db_latch (.EN(PHI2), .D(nor_19_out), .NOT_Q(sb_db_latch_not_q));  // open: Q
  D_Latch ac_db_latch (.EN(PHI2), .D(nor_4_out), .Q(ac_db_latch_q));  // open: NOT_Q
  D_Latch sb_adh_latch (.EN(PHI2), .D(nor_12_out), .NOT_Q(sb_adh_latch_not_q));  // open: Q
  D_Latch dl_adh_latch (.EN(PHI2), .D(nor_20_out), .NOT_Q(dl_adh_latch_not_q));  // open: Q
  D_Latch dl_adl_latch (.EN(PHI2), .D(nor_2_out), .NOT_Q(dl_adl_latch_not_q));  // open: Q
  D_Latch adh_abh_latch (.EN(PHI2), .D(nor_21_out), .NOT_Q(adh_abh_latch_not_q));  // open: Q
  D_Latch dl_db_latch (.EN(PHI2), .D(nor_22_out), .NOT_Q(dl_db_latch_not_q));  // open: Q
  buf buffer_1 (_0_ADH17, z_adh17_latch_not_q);
  buf buffer_2 (SB_AC, nor_23_out);
  nor nor_23 (nor_23_out, sb_ac_latch_q, PHI2);
  not not_10 (ZTST, nor_10_out);
  buf buffer_3 (ADL_ABL, adl_abl_latch_not_q);
  buf buffer_4 (AC_SB, nor_24_out);
  nor nor_24 (nor_24_out, ac_sb_latch_q, PHI2);
  buf buffer_5 (SB_DB, sb_db_latch_not_q);
  buf buffer_6 (AC_DB, nor_25_out);
  nor nor_25 (nor_25_out, ac_db_latch_q, PHI2);
  buf buffer_7 (SB_ADH, sb_adh_latch_not_q);
  buf buffer_8 (DL_ADH, dl_adh_latch_not_q);
  buf buffer_9 (DL_ADL, dl_adl_latch_not_q);
  buf buffer_10 (ADH_ABH, adh_abh_latch_not_q);
  buf buffer_11 (DL_DB, dl_db_latch_not_q);

  // Other names for the same wires on the sheet: RTS_5 = D84

  // Notes on the sheet:
  //   BR0
  //   STA
  //   push/pull
  //   JSR2
  //   #DL/ADL
  //   ABS/2
  //   #SB/AC
  //   PGX
  //   IMPLIED
  //   JSR/5
  //   SBXY
  //   AND
  //   IND
  //   #DL/ADL
  //   #ZTST
  //   SBA
  //   JSXY
  //   JSXY
  //   JMP/4
  //   #DL/ADL
  //   #SB/AC
  //   #ADL/ABL
  //   #AC/SB
  //   #SB/DB
  //   #DL/ADL
  //   #DL/DB
endmodule

// FLAGS CONTROL
module FLAGS_CONTROL (
  input  PHI2,
  input  D98,
  input  D99,
  input  D108,
  input  D110,
  input  D120,
  input  D127,
  input  D107,
  input  T6,
  input  D112,
  input  D116,
  input  D117,
  input  D118,
  input  D119,
  input  ZTST,
  input  D109,
  input  nready,
  input  SR,
  input  D114,
  input  D115,
  input  D113,
  output P_DB,
  output IR5_I,
  output IR5_C,
  output IR5_D,
  output _0_V,
  output ACR_C,
  output DBZ_Z,
  output DB_N,
  output DB_P,
  output DB_C,
  output DB_V
);

  wire and_1_out, and_2_out, bit_latch_q, dbn_latch_q, dbz_latch_q, nor_1_out, nor_2_out, nor_3_out,
       nor_4_out, nor_5_out, not_1_out, not_2_out, not_3_out, not_4_out, not_5_out, pin_latch_q;

  and and_1 (and_1_out, D107, T6);
  nor nor_1 (nor_1_out, D98, D99);
  not not_1 (not_1_out, D108);
  not not_2 (not_2_out, D110);
  not not_3 (not_3_out, D120);
  not not_4 (not_4_out, D127);
  nor nor_2 (nor_2_out, D114, D115);
  not not_5 (not_5_out, D113);
  nor nor_3 (nor_3_out, and_1_out, D112, D116, D117, D118, D119);
  nor nor_4 (nor_4_out, ACR_C, ZTST, D109);
  nor nor_5 (nor_5_out, SR, DB_P);
  D_Latch pdb_latch (.EN(PHI2), .D(nor_1_out), .NOT_Q(P_DB));  // open: Q
  D_Latch iri_latch (.EN(PHI2), .D(not_1_out), .NOT_Q(IR5_I));  // open: Q
  D_Latch irc_latch (.EN(PHI2), .D(not_2_out), .NOT_Q(IR5_C));  // open: Q
  D_Latch ird_latch (.EN(PHI2), .D(not_3_out), .NOT_Q(IR5_D));  // open: Q
  D_Latch zv_latch (.EN(PHI2), .D(not_4_out), .NOT_Q(_0_V));  // open: Q
  D_Latch acrc_latch (.EN(PHI2), .D(nor_3_out), .NOT_Q(ACR_C));  // open: Q
  D_Latch dbz_latch (.EN(PHI2), .D(nor_4_out), .Q(dbz_latch_q), .NOT_Q(DBZ_Z));
  D_Latch dbn_latch (.EN(PHI2), .D(D109), .Q(dbn_latch_q));  // open: NOT_Q
  D_Latch dbc_latch (.EN(PHI2), .D(nor_5_out), .NOT_Q(DB_C));  // open: Q
  D_Latch pin_latch (.EN(PHI2), .D(nor_2_out), .Q(pin_latch_q));  // open: NOT_Q
  D_Latch bit_latch (.EN(PHI2), .D(not_5_out), .Q(bit_latch_q));  // open: NOT_Q
  and and_2 (and_2_out, dbz_latch_q, pin_latch_q);
  nor nor_6 (DB_N, and_2_out, dbn_latch_q);
  nor nor_7 (DB_P, pin_latch_q, nready);
  nand nand_1 (DB_V, pin_latch_q, bit_latch_q);

  // Notes on the sheet:
  //   AVR/V
  //   BIT1
  //   BIT0
  //   /POUT
  //   /CSI
  //   ZTST
  //   /PIN
  //   /ARIT
  //   BIT1
endmodule

module FLAGS (
  input  P_DB,
  input  B_OUT,
  input  DB0,
  input  DB1,
  input  DB2,
  input  DB3,
  input  DB4,
  input  DB5,
  input  DB6,
  input  DB7,
  input  DB_P,
  input  DBZ_Z,
  input  DB_N,
  input  IR5_C,
  input  ACR,
  input  DB_C,
  input  ACR_C,
  input  IR5_D,
  input  PHI1,
  input  PHI2,
  input  nIR5,
  input  IR5_I,
  input  BRK6E,
  input  AVR,
  input  DB_V,
  input  D112,
  input  _0_V,
  input  SO,
  output DB0_2,
  output DB1_2,
  output DB2_2,
  output DB3_2,
  output DB4_2,
  output DB5_2,
  output DB6_2,
  output DB7_2,
  output nZ_OUT,
  output nN_OUT,
  output nC_OUT,
  output nD_OUT,
  output nI_OUT,
  output nV_OUT
);

  wire and_1_out, and_2_out, and_3_out, and_4_out, and_5_out, and_6_out, and_7_out, and_8_out, and_9_out,
       and_10_out, and_11_out, and_12_out, and_13_out, and_14_out, and_15_out, and_16_out, and_17_out,
       and_18_out, avr_latch_q, c_latch2_q, d_latch2_q, i_latch1_not_q, i_latch2_q, n_latch2_q, nor_1_out,
       nor_2_out, nor_3_out, nor_4_out, nor_5_out, nor_6_out, nor_7_out, nor_8_out, nor_9_out, nor_10_out,
       nor_11_out, nor_12_out, nor_13_out, not_1_out, not_2_out, not_3_out, not_4_out, not_5_out, not_6_out,
       not_7_out, not_8_out, not_9_out, not_10_out, not_11_out, not_12_out, not_13_out, not_14_out,
       not_15_out, not_16_out, not_17_out, so_latch1_not_q, so_latch2_not_q, so_latch3_q, v_latch2_q,
       vset_latch_q, z_latch2_q;

  D_Latch avr_latch (.EN(PHI2), .D(D112), .Q(avr_latch_q));  // open: NOT_Q
  not not_1 (not_1_out, SO);
  nor nor_1 (nor_1_out, DB0, DB1, DB2, DB3, DB4, DB5, DB6, DB7);
  not not_2 (not_2_out, DB1);
  not not_3 (not_3_out, nor_1_out);
  not not_4 (not_4_out, DB7);
  nor nor_2 (nor_2_out, DB_P, DBZ_Z);
  not not_5 (not_5_out, DB_N);
  not not_6 (not_6_out, ACR);
  not not_7 (not_7_out, DB0);
  nor nor_3 (nor_3_out, DB_C, IR5_C, ACR_C);
  not not_8 (not_8_out, DB3);
  nor nor_4 (nor_4_out, IR5_D, DB_P);
  not not_9 (not_9_out, DB2);
  nor nor_5 (nor_5_out, DB_P, IR5_I);
  not not_10 (not_10_out, AVR);
  not not_11 (not_11_out, DB6);
  nor nor_6 (nor_6_out, DB_V, avr_latch_q, vset_latch_q);
  D_Latch so_latch1 (.EN(PHI1), .D(not_1_out), .NOT_Q(so_latch1_not_q));  // open: Q
  and and_1 (and_1_out, not_2_out, DB_P);
  and and_2 (and_2_out, not_3_out, DBZ_Z);
  and and_3 (and_3_out, nor_2_out, z_latch2_q);
  and and_4 (and_4_out, not_4_out, DB_N);
  and and_5 (and_5_out, not_5_out, n_latch2_q);
  and and_6 (and_6_out, nIR5, IR5_C);
  and and_7 (and_7_out, not_6_out, ACR_C);
  and and_8 (and_8_out, not_7_out, DB_C);
  and and_9 (and_9_out, nor_3_out, c_latch2_q);
  and and_10 (and_10_out, IR5_D, nIR5);
  and and_11 (and_11_out, not_8_out, DB_P);
  and and_12 (and_12_out, nor_4_out, d_latch2_q);
  and and_13 (and_13_out, nIR5, IR5_I);
  and and_14 (and_14_out, not_9_out, DB_P);
  and and_15 (and_15_out, nor_5_out, i_latch2_q);
  and and_16 (and_16_out, not_10_out, avr_latch_q);
  and and_17 (and_17_out, not_11_out, DB_V);
  and and_18 (and_18_out, nor_6_out, v_latch2_q);
  D_Latch so_latch2 (.EN(PHI2), .D(so_latch1_not_q), .NOT_Q(so_latch2_not_q));  // open: Q
  nor nor_7 (nor_7_out, and_1_out, and_2_out, and_3_out);
  nor nor_8 (nor_8_out, and_4_out, and_5_out);
  nor nor_9 (nor_9_out, and_6_out, and_7_out, and_8_out, and_9_out);
  nor nor_10 (nor_10_out, and_10_out, and_11_out, and_12_out);
  nor nor_11 (nor_11_out, and_13_out, and_14_out, and_15_out);
  nor nor_12 (nor_12_out, and_16_out, and_17_out, and_18_out, _0_V);
  D_Latch so_latch3 (.EN(PHI1), .D(so_latch2_not_q), .Q(so_latch3_q));  // open: NOT_Q
  nor nor_13 (nor_13_out, so_latch3_q, so_latch1_not_q);
  D_Latch z_latch1 (.EN(PHI1), .D(nor_7_out), .NOT_Q(nZ_OUT));  // open: Q
  D_Latch z_latch2 (.EN(PHI2), .D(nZ_OUT), .Q(z_latch2_q));  // open: NOT_Q
  D_Latch n_latch1 (.EN(PHI1), .D(nor_8_out), .NOT_Q(nN_OUT));  // open: Q
  D_Latch n_latch2 (.EN(PHI2), .D(nN_OUT), .Q(n_latch2_q));  // open: NOT_Q
  D_Latch c_latch1 (.EN(PHI1), .D(nor_9_out), .NOT_Q(nC_OUT));  // open: Q
  D_Latch c_latch2 (.EN(PHI2), .D(nC_OUT), .Q(c_latch2_q));  // open: NOT_Q
  D_Latch d_latch1 (.EN(PHI1), .D(nor_10_out), .NOT_Q(nD_OUT));  // open: Q
  D_Latch d_latch2 (.EN(PHI2), .D(nD_OUT), .Q(d_latch2_q));  // open: NOT_Q
  D_Latch i_latch1 (.EN(PHI1), .D(nor_11_out), .NOT_Q(i_latch1_not_q));  // open: Q
  D_Latch i_latch2 (.EN(PHI2), .D(nI_OUT), .Q(i_latch2_q));  // open: NOT_Q
  D_Latch v_latch1 (.EN(PHI1), .D(nor_12_out), .NOT_Q(nV_OUT));  // open: Q
  D_Latch v_latch2 (.EN(PHI2), .D(nV_OUT), .Q(v_latch2_q));  // open: NOT_Q
  D_Latch vset_latch (.EN(PHI2), .D(nor_13_out), .Q(vset_latch_q));  // open: NOT_Q
  and and_19 (nI_OUT, ~BRK6E, i_latch1_not_q);  // AND_Gate
  assign DB0_2 = P_DB ? not_12_out : 1'bz;  // Controlled_Buffer controlled_buffer_1
  not not_12 (not_12_out, nC_OUT);
  not not_13 (not_13_out, nZ_OUT);
  assign DB1_2 = P_DB ? not_13_out : 1'bz;  // Controlled_Buffer controlled_buffer_2
  not not_14 (not_14_out, nI_OUT);
  assign DB2_2 = P_DB ? not_14_out : 1'bz;  // Controlled_Buffer controlled_buffer_3
  not not_15 (not_15_out, nD_OUT);
  assign DB3_2 = P_DB ? not_15_out : 1'bz;  // Controlled_Buffer controlled_buffer_4
  assign DB4_2 = P_DB ? B_OUT : 1'bz;  // Controlled_Buffer controlled_buffer_5
  assign DB6_2 = P_DB ? not_16_out : 1'bz;  // Controlled_Buffer controlled_buffer_6
  not not_16 (not_16_out, nV_OUT);
  assign DB7_2 = P_DB ? not_17_out : 1'bz;  // Controlled_Buffer controlled_buffer_7
  not not_17 (not_17_out, nN_OUT);

  // Notes on the sheet:
  //   AVR/V
  //   ACR/C
  //   /DB1
  //   /DBZ
  //   /DB7
  //   DB/C
  //   IR5/D
  //   IR5/I
  //   DB/V
  //   1/V
  //   IR5/C
  //   /ACR
  //   ACR/C
  //   /DB0
  //   DB/C
  //   IR5/D
  //   /DB3
  //   IR5/I
  //   /DB2
  //   /AVR
  //   /DB6
  //   DB/V
  //   0/V
  //   Z FLAG
  //   /Z_OUT
  //   N FLAG
  //   /N_OUT
  //   C FLAG
  //   /C_OUT
  //   D FLAG
  //   /D_OUT
  //   I FLAG
  //   V FLAG
  //   /V_OUT
  //   /I_OUT
  //   N.C.
endmodule

module ABH (
  input  PHI1,
  input  PHI2,
  input  ADH_ABH,
  input  ADH0,
  input  ADH1,
  input  ADH2,
  input  ADH3,
  input  ADH4,
  input  ADH5,
  input  ADH6,
  input  ADH7,
  output A8,
  output A9,
  output A10,
  output A11,
  output A12,
  output A13,
  output A14,
  output A15
);

  ABH_BIT _0 (.PHI1(PHI1), .PHI2(PHI2), .ADH_ABH(ADH_ABH), .ADHx(ADH0), .Ax(A8));
  ABH_BIT _1 (.PHI1(PHI1), .PHI2(PHI2), .ADH_ABH(ADH_ABH), .ADHx(ADH1), .Ax(A9));
  ABH_BIT _2 (.PHI1(PHI1), .PHI2(PHI2), .ADH_ABH(ADH_ABH), .ADHx(ADH2), .Ax(A10));
  ABH_BIT _3 (.PHI1(PHI1), .PHI2(PHI2), .ADH_ABH(ADH_ABH), .ADHx(ADH3), .Ax(A11));
  ABH_BIT _4 (.PHI1(PHI1), .PHI2(PHI2), .ADH_ABH(ADH_ABH), .ADHx(ADH4), .Ax(A12));
  ABH_BIT _5 (.PHI1(PHI1), .PHI2(PHI2), .ADH_ABH(ADH_ABH), .ADHx(ADH5), .Ax(A13));
  ABH_BIT _6 (.PHI1(PHI1), .PHI2(PHI2), .ADH_ABH(ADH_ABH), .ADHx(ADH6), .Ax(A14));
  ABH_BIT _7 (.PHI1(PHI1), .PHI2(PHI2), .ADH_ABH(ADH_ABH), .ADHx(ADH7), .Ax(A15));
endmodule

module ABL (
  input  PHI1,
  input  PHI2,
  input  ADL_ABL,
  input  ADL0,
  input  ADL1,
  input  ADL2,
  input  ADL3,
  input  ADL4,
  input  ADL5,
  input  ADL6,
  input  ADL7,
  output A0,
  output A1,
  output A2,
  output A3,
  output A4,
  output A5,
  output A6,
  output A7
);

  ABL_BIT _0 (.PHI1(PHI1), .PHI2(PHI2), .ADL_ABL(ADL_ABL), .ADLx(ADL0), .Ax(A0));
  ABL_BIT _1 (.PHI1(PHI1), .PHI2(PHI2), .ADL_ABL(ADL_ABL), .ADLx(ADL1), .Ax(A1));
  ABL_BIT _2 (.PHI1(PHI1), .PHI2(PHI2), .ADL_ABL(ADL_ABL), .ADLx(ADL2), .Ax(A2));
  ABL_BIT _3 (.PHI1(PHI1), .PHI2(PHI2), .ADL_ABL(ADL_ABL), .ADLx(ADL3), .Ax(A3));
  ABL_BIT _4 (.PHI1(PHI1), .PHI2(PHI2), .ADL_ABL(ADL_ABL), .ADLx(ADL4), .Ax(A4));
  ABL_BIT _5 (.PHI1(PHI1), .PHI2(PHI2), .ADL_ABL(ADL_ABL), .ADLx(ADL5), .Ax(A5));
  ABL_BIT _6 (.PHI1(PHI1), .PHI2(PHI2), .ADL_ABL(ADL_ABL), .ADLx(ADL6), .Ax(A6));
  ABL_BIT _7 (.PHI1(PHI1), .PHI2(PHI2), .ADL_ABL(ADL_ABL), .ADLx(ADL7), .Ax(A7));
endmodule

module REGS_BIT (
  input  PHI2,
  input  Y_SB,
  input  SB_Y,
  input  X_SB,
  input  SB_X,
  input  S_ADL,
  input  S_S,
  input  SB_S,
  input  S_SB,
  input  SBx,
  output SBx_2,
  output ADLx,
  output Y_Debug,
  output X_Debug,
  output S_Debug
);

  wire and_1_out, and_2_out, multiplexer_1_out, not_1_out, not_2_out, not_3_out, S_in_not_q;

  not not_1 (not_1_out, PHI2);
  not not_2 (not_2_out, PHI2);
  not not_3 (not_3_out, PHI2);
  DFF_Level Y (.EN(and_1_out), .D(SBx), .Q(Y_Debug));  // open: NOT_Q
  and and_1 (and_1_out, not_1_out, SB_Y);
  and and_2 (and_2_out, not_2_out, SB_X);
  DFF_Level X (.EN(and_2_out), .D(SBx), .Q(X_Debug));  // open: NOT_Q
  Multiplexer multiplexer_1 (.in0(S_Debug), .in1(SBx), .out(multiplexer_1_out), .sel(SB_S));  // open: en
  D_Latch S_in (.EN(not_3_out), .D(multiplexer_1_out), .NOT_Q(S_in_not_q));  // open: Q
  D_Latch S_out (.EN(PHI2), .D(S_in_not_q), .NOT_Q(S_Debug));  // open: Q
  assign SBx_2 = Y_SB ? Y_Debug : 1'bz;  // Controlled_Buffer controlled_buffer_1
  assign SBx_2 = X_SB ? X_Debug : 1'bz;  // Controlled_Buffer controlled_buffer_2
  assign SBx_2 = S_SB ? S_Debug : 1'bz;  // Controlled_Buffer controlled_buffer_3
  assign ADLx = S_ADL ? S_Debug : 1'bz;  // Controlled_Buffer controlled_buffer_4

  // Notes on the sheet:
  //   unused
endmodule

module REGS (
  input  PHI2,
  input  Y_SB,
  input  SB_Y,
  input  X_SB,
  input  SB_X,
  input  S_ADL,
  input  S_S,
  input  SB_S,
  input  S_SB,
  input  SB0,
  input  SB1,
  input  SB2,
  input  SB3,
  input  SB4,
  input  SB5,
  input  SB6,
  input  SB7,
  output SB0_2,
  output SB1_2,
  output SB2_2,
  output SB3_2,
  output SB4_2,
  output SB5_2,
  output SB6_2,
  output SB7_2,
  output ADL0,
  output ADL1,
  output ADL2,
  output ADL3,
  output ADL4,
  output ADL5,
  output ADL6,
  output ADL7,
  output [7:0] S_Debug,
  output [7:0] Y_Debug,
  output [7:0] X_Debug
);

  REGS_BIT _0 (
    .PHI2(PHI2), .Y_SB(Y_SB), .SB_Y(SB_Y), .X_SB(X_SB), .SB_X(SB_X), .S_ADL(S_ADL), .S_S(S_S), .SB_S(SB_S),
    .S_SB(S_SB), .SBx(SB0), .SBx_2(SB0_2), .ADLx(ADL0), .Y_Debug(Y_Debug[0]), .X_Debug(X_Debug[0]),
    .S_Debug(S_Debug[0]));
  REGS_BIT _4 (
    .PHI2(PHI2), .Y_SB(Y_SB), .SB_Y(SB_Y), .X_SB(X_SB), .SB_X(SB_X), .S_ADL(S_ADL), .S_S(S_S), .SB_S(SB_S),
    .S_SB(S_SB), .SBx(SB4), .SBx_2(SB4_2), .ADLx(ADL4), .Y_Debug(Y_Debug[4]), .X_Debug(X_Debug[4]),
    .S_Debug(S_Debug[4]));
  REGS_BIT _1 (
    .PHI2(PHI2), .Y_SB(Y_SB), .SB_Y(SB_Y), .X_SB(X_SB), .SB_X(SB_X), .S_ADL(S_ADL), .S_S(S_S), .SB_S(SB_S),
    .S_SB(S_SB), .SBx(SB1), .SBx_2(SB1_2), .ADLx(ADL1), .Y_Debug(Y_Debug[1]), .X_Debug(X_Debug[1]),
    .S_Debug(S_Debug[1]));
  REGS_BIT _5 (
    .PHI2(PHI2), .Y_SB(Y_SB), .SB_Y(SB_Y), .X_SB(X_SB), .SB_X(SB_X), .S_ADL(S_ADL), .S_S(S_S), .SB_S(SB_S),
    .S_SB(S_SB), .SBx(SB5), .SBx_2(SB5_2), .ADLx(ADL5), .Y_Debug(Y_Debug[5]), .X_Debug(X_Debug[5]),
    .S_Debug(S_Debug[5]));
  REGS_BIT _2 (
    .PHI2(PHI2), .Y_SB(Y_SB), .SB_Y(SB_Y), .X_SB(X_SB), .SB_X(SB_X), .S_ADL(S_ADL), .S_S(S_S), .SB_S(SB_S),
    .S_SB(S_SB), .SBx(SB2), .SBx_2(SB2_2), .ADLx(ADL2), .Y_Debug(Y_Debug[2]), .X_Debug(X_Debug[2]),
    .S_Debug(S_Debug[2]));
  REGS_BIT _6 (
    .PHI2(PHI2), .Y_SB(Y_SB), .SB_Y(SB_Y), .X_SB(X_SB), .SB_X(SB_X), .S_ADL(S_ADL), .S_S(S_S), .SB_S(SB_S),
    .S_SB(S_SB), .SBx(SB6), .SBx_2(SB6_2), .ADLx(ADL6), .Y_Debug(Y_Debug[6]), .X_Debug(X_Debug[6]),
    .S_Debug(S_Debug[6]));
  REGS_BIT _3 (
    .PHI2(PHI2), .Y_SB(Y_SB), .SB_Y(SB_Y), .X_SB(X_SB), .SB_X(SB_X), .S_ADL(S_ADL), .S_S(S_S), .SB_S(SB_S),
    .S_SB(S_SB), .SBx(SB3), .SBx_2(SB3_2), .ADLx(ADL3), .Y_Debug(Y_Debug[3]), .X_Debug(X_Debug[3]),
    .S_Debug(S_Debug[3]));
  REGS_BIT _7 (
    .PHI2(PHI2), .Y_SB(Y_SB), .SB_Y(SB_Y), .X_SB(X_SB), .SB_X(SB_X), .S_ADL(S_ADL), .S_S(S_S), .SB_S(SB_S),
    .S_SB(S_SB), .SBx(SB7), .SBx_2(SB7_2), .ADLx(ADL7), .Y_Debug(Y_Debug[7]), .X_Debug(X_Debug[7]),
    .S_Debug(S_Debug[7]));
endmodule

module DL_BIT (
  input  PHI1,
  input  PHI2,
  input  DL_ADL,
  input  DL_ADH,
  input  DL_DB,
  input  RD,
  input  DBx,
  input  Dx,
  output ADLx,
  output ADHx,
  output DBx_2,
  output Dx_2,
  output DOR_Debug,
  output DL_Debug
);

  wire and_1_out, and_2_out, and_3_out, not_1_out, not_2_out, not_3_out;

  D_Latch DL (.EN(PHI2), .D(not_1_out), .NOT_Q(DL_Debug));  // open: Q
  not not_1 (not_1_out, Dx);
  D_Latch DOR (.EN(PHI1), .D(not_2_out), .NOT_Q(DOR_Debug));  // open: Q
  not not_2 (not_2_out, DBx);
  and and_1 (and_1_out, DL_ADL, PHI1);
  and and_2 (and_2_out, DL_ADH, PHI1);
  and and_3 (and_3_out, DL_DB, PHI1);
  not not_3 (not_3_out, RD);
  assign ADLx = and_1_out ? DL_Debug : 1'bz;  // Controlled_Buffer controlled_buffer_1
  assign ADHx = and_2_out ? DL_Debug : 1'bz;  // Controlled_Buffer controlled_buffer_2
  assign DBx_2 = and_3_out ? DL_Debug : 1'bz;  // Controlled_Buffer controlled_buffer_3
  assign Dx_2 = not_3_out ? DOR_Debug : 1'bz;  // Controlled_Buffer controlled_buffer_4
endmodule

module DL (
  input  PHI1,
  input  PHI2,
  input  WR,
  input  DL_ADL,
  input  DL_ADH,
  input  DL_DB,
  input  DB0,
  input  DB1,
  input  DB2,
  input  DB3,
  input  DB4,
  input  DB5,
  input  DB6,
  input  DB7,
  input  D0,
  input  D1,
  input  D2,
  input  D3,
  input  D4,
  input  D5,
  input  D6,
  input  D7,
  output DB0_2,
  output DB1_2,
  output DB2_2,
  output DB3_2,
  output DB4_2,
  output DB5_2,
  output DB6_2,
  output DB7_2,
  output ADL0,
  output ADL1,
  output ADL2,
  output ADL3,
  output ADL4,
  output ADL5,
  output ADL6,
  output ADL7,
  output ADH0,
  output ADH1,
  output ADH2,
  output ADH3,
  output ADH4,
  output ADH5,
  output ADH6,
  output ADH7,
  output D0_2,
  output D1_2,
  output D2_2,
  output D3_2,
  output D4_2,
  output D5_2,
  output D6_2,
  output D7_2,
  output [7:0] DL_Debug,
  output [7:0] DOR_Debug
);

  wire d_latch_1_not_q, RD;

  D_Latch d_latch_1 (.EN(PHI1), .D(WR), .NOT_Q(d_latch_1_not_q));  // open: Q
  Multiplexer #(.enable("false")) multiplexer_1 (.in0(d_latch_1_not_q), .in1(1'b1), .out(RD), .sel(PHI2));
  DL_BIT _0 (
    .PHI1(PHI1), .PHI2(PHI2), .DL_ADL(DL_ADL), .DL_ADH(DL_ADH), .DL_DB(DL_DB), .RD(RD), .DBx(DB0), .Dx(D0),
    .DBx_2(DB0_2), .ADLx(ADL0), .ADHx(ADH0), .Dx_2(D0_2), .DOR_Debug(DOR_Debug[0]), .DL_Debug(DL_Debug[0]));
  DL_BIT _1 (
    .PHI1(PHI1), .PHI2(PHI2), .DL_ADL(DL_ADL), .DL_ADH(DL_ADH), .DL_DB(DL_DB), .RD(RD), .DBx(DB1), .Dx(D1),
    .DBx_2(DB1_2), .ADLx(ADL1), .ADHx(ADH1), .Dx_2(D1_2), .DOR_Debug(DOR_Debug[1]), .DL_Debug(DL_Debug[1]));
  DL_BIT _2 (
    .PHI1(PHI1), .PHI2(PHI2), .DL_ADL(DL_ADL), .DL_ADH(DL_ADH), .DL_DB(DL_DB), .RD(RD), .DBx(DB2), .Dx(D2),
    .DBx_2(DB2_2), .ADLx(ADL2), .ADHx(ADH2), .Dx_2(D2_2), .DOR_Debug(DOR_Debug[2]), .DL_Debug(DL_Debug[2]));
  DL_BIT _3 (
    .PHI1(PHI1), .PHI2(PHI2), .DL_ADL(DL_ADL), .DL_ADH(DL_ADH), .DL_DB(DL_DB), .RD(RD), .DBx(DB3), .Dx(D3),
    .DBx_2(DB3_2), .ADLx(ADL3), .ADHx(ADH3), .Dx_2(D3_2), .DOR_Debug(DOR_Debug[3]), .DL_Debug(DL_Debug[3]));
  DL_BIT _4 (
    .PHI1(PHI1), .PHI2(PHI2), .DL_ADL(DL_ADL), .DL_ADH(DL_ADH), .DL_DB(DL_DB), .RD(RD), .DBx(DB4), .Dx(D4),
    .DBx_2(DB4_2), .ADLx(ADL4), .ADHx(ADH4), .Dx_2(D4_2), .DOR_Debug(DOR_Debug[4]), .DL_Debug(DL_Debug[4]));
  DL_BIT _5 (
    .PHI1(PHI1), .PHI2(PHI2), .DL_ADL(DL_ADL), .DL_ADH(DL_ADH), .DL_DB(DL_DB), .RD(RD), .DBx(DB5), .Dx(D5),
    .DBx_2(DB5_2), .ADLx(ADL5), .ADHx(ADH5), .Dx_2(D5_2), .DOR_Debug(DOR_Debug[5]), .DL_Debug(DL_Debug[5]));
  DL_BIT _6 (
    .PHI1(PHI1), .PHI2(PHI2), .DL_ADL(DL_ADL), .DL_ADH(DL_ADH), .DL_DB(DL_DB), .RD(RD), .DBx(DB6), .Dx(D6),
    .DBx_2(DB6_2), .ADLx(ADL6), .ADHx(ADH6), .Dx_2(D6_2), .DOR_Debug(DOR_Debug[6]), .DL_Debug(DL_Debug[6]));
  DL_BIT _7 (
    .PHI1(PHI1), .PHI2(PHI2), .DL_ADL(DL_ADL), .DL_ADH(DL_ADH), .DL_DB(DL_DB), .RD(RD), .DBx(DB7), .Dx(D7),
    .DBx_2(DB7_2), .ADLx(ADL7), .ADHx(ADH7), .Dx_2(D7_2), .DOR_Debug(DOR_Debug[7]), .DL_Debug(DL_Debug[7]));
endmodule

module ALU (
  input  PHI2,
  input  NDB_ADD,
  input  DB_ADD,
  input  _0_ADD,
  input  SB_ADD,
  input  ADL_ADD,
  input  ADD_SB06,
  input  ADD_SB7,
  input  ADD_ADL,
  input  ANDS,
  input  EORS,
  input  SB_Dirty,
  input  ORS,
  input  DB_Dirty,
  input  SRS,
  input  ADH_Dirty,
  input  SUMS,
  input  SB_AC,
  input  AC_SB,
  input  AC_DB,
  input  SB_DB,
  input  SB_ADH,
  input  nACIN,
  input  nDAA,
  input  nDSA,
  input  SB0,
  input  DB0,
  input  [7:0] ADL_In,
  input  SB1,
  input  DB1,
  input  [7:0] ADH_In,
  input  SB2,
  input  DB2,
  input  SB3,
  input  DB3,
  input  SB4,
  input  DB4,
  input  SB5,
  input  DB5,
  input  SB6,
  input  DB6,
  input  SB7,
  input  DB7,
  output ACR,
  output AVR,
  output [7:0] ADD_Debug,
  output [7:0] AC_Debug,
  output [7:0] AI_Debug,
  output [7:0] BI_Debug,
  output SB0_2,
  output DB0_2,
  output ADL0,
  output ADH0,
  output SB1_2,
  output DB1_2,
  output ADL1,
  output ADH1,
  output SB2_2,
  output DB2_2,
  output ADL2,
  output ADH2,
  output SB3_2,
  output DB3_2,
  output ADL3,
  output ADH3,
  output SB4_2,
  output DB4_2,
  output ADL4,
  output ADH4,
  output SB5_2,
  output DB5_2,
  output ADL5,
  output ADH5,
  output SB6_2,
  output DB6_2,
  output ADL6,
  output ADH6,
  output SB7_2,
  output DB7_2,
  output ADL7,
  output ADH7
);

  wire ACLatch_q, alu_ops_1_carry4, alu_ops_1_carry6, alu_ops_1_ncarry3, alu_ops_1_ncarry7, and_1_out,
       bcd_carry_1_dc3, bcd_carry_1_dc7, DCLatch_q, nand_1_out, nor_1_out, nor_2_out, not_1_out, not_2_out;
  wire [7:0] alu_add_1_naddx, alu_bcd_1_out0, alu_ops_1_nand0, alu_ops_1_nor0, alu_ops_1_res0, alu_ops_1_xor0;

  ALU_OPS alu_ops_1 (
    .NDB_ADD(NDB_ADD), .DB_ADD(DB_ADD), ._0_ADD(_0_ADD), .SB_ADD(SB_ADD), .ADL_ADD(ADL_ADD), .ANDS(ANDS),
    .EORS(EORS), .ORS(ORS), .SRS(SRS), .SUMS(SUMS), .ncin(nACIN), .res0(alu_ops_1_res0[0]),
    .ncarry7(alu_ops_1_ncarry7), .SB0(SB0), .SB1(SB1), .SB2(SB2), .SB3(SB3), .SB4(SB4), .SB5(SB5), .SB6(SB6),
    .SB7(SB7), .DB0(DB0), .DB1(DB1), .DB2(DB2), .DB3(DB3), .DB4(DB4), .DB5(DB5), .DB6(DB6), .DB7(DB7),
    .ADL0(ADL_In[0]), .ADL1(ADL_In[1]), .ADL2(ADL_In[2]), .ADL3(ADL_In[3]), .ADL4(ADL_In[4]),
    .ADL5(ADL_In[5]), .ADL6(ADL_In[6]), .ADL7(ADL_In[7]), .res1(alu_ops_1_res0[1]), .res2(alu_ops_1_res0[2]),
    .res3(alu_ops_1_res0[3]), .res4(alu_ops_1_res0[4]), .res5(alu_ops_1_res0[5]), .res6(alu_ops_1_res0[6]),
    .res7(alu_ops_1_res0[7]), .nor0(alu_ops_1_nor0[0]), .nor1(alu_ops_1_nor0[1]), .nor2(alu_ops_1_nor0[2]),
    .nor3(alu_ops_1_nor0[3]), .nor4(alu_ops_1_nor0[4]), .nor5(alu_ops_1_nor0[5]), .nor6(alu_ops_1_nor0[6]),
    .nor7(alu_ops_1_nor0[7]), .nand0(alu_ops_1_nand0[0]), .nand1(alu_ops_1_nand0[1]),
    .nand2(alu_ops_1_nand0[2]), .nand3(alu_ops_1_nand0[3]), .nand4(alu_ops_1_nand0[4]),
    .nand5(alu_ops_1_nand0[5]), .nand6(alu_ops_1_nand0[6]), .nand7(alu_ops_1_nand0[7]),
    .xor0(alu_ops_1_xor0[0]), .xor1(alu_ops_1_xor0[1]), .xor2(alu_ops_1_xor0[2]), .xor3(alu_ops_1_xor0[3]),
    .xor4(alu_ops_1_xor0[4]), .xor5(alu_ops_1_xor0[5]), .xor6(alu_ops_1_xor0[6]), .xor7(alu_ops_1_xor0[7]),
    .AI_Debug(AI_Debug), .BI_Debug(BI_Debug), .DC3(bcd_carry_1_dc3), .carry6(alu_ops_1_carry6),
    .ncarry3(alu_ops_1_ncarry3), .carry4(alu_ops_1_carry4));
  BCD_CARRY bcd_carry_1 (
    .nACIN(nACIN), .carry4(alu_ops_1_carry4), .\nor (alu_ops_1_nor0), .\nand (alu_ops_1_nand0),
    .\xor (alu_ops_1_xor0), .DC3(bcd_carry_1_dc3), .DC7(bcd_carry_1_dc7), .nDAA(nDAA));
  nand nand_1 (nand_1_out, alu_ops_1_carry6, alu_ops_1_nor0[7]);
  nor nor_1 (nor_1_out, alu_ops_1_carry6, alu_ops_1_ncarry7);
  not not_1 (not_1_out, alu_ops_1_ncarry7);
  and and_1 (and_1_out, nand_1_out, not_2_out);
  not not_2 (not_2_out, nor_1_out);
  ALU_ADD alu_add_1 (
    .PHI2(PHI2), .ADD_SB06(ADD_SB06), .ADD_SB7(ADD_SB7), .ADD_ADL(ADD_ADL), .nres(alu_ops_1_res0),
    .nADDx(alu_add_1_naddx), .SB0(SB0_2), .SB1(SB1_2), .SB2(SB2_2), .SB3(SB3_2), .SB4(SB4_2), .SB5(SB5_2),
    .SB6(SB6_2), .SB7(SB7_2), .ADL0(ADL0), .ADL1(ADL1), .ADL2(ADL2), .ADL3(ADL3), .ADL4(ADL4), .ADL5(ADL5),
    .ADL6(ADL6), .ADL7(ADL7), .ADD_Debug(ADD_Debug));
  D_Latch DCLatch (.EN(PHI2), .D(bcd_carry_1_dc7), .Q(DCLatch_q));  // open: NOT_Q
  D_Latch ACLatch (.EN(PHI2), .D(not_1_out), .Q(ACLatch_q));  // open: NOT_Q
  D_Latch AVRLatch (.EN(PHI2), .D(and_1_out), .NOT_Q(AVR));  // open: Q
  nor nor_2 (nor_2_out, DCLatch_q, ACLatch_q);
  not not_3 (ACR, nor_2_out);
  ALU_BCD alu_bcd_1 (
    .PHI2(PHI2), .ACR(ACR), .nDAA(nDAA), .nDSA(nDSA), .SB0(SB0), .SB1(SB1), .SB2(SB2), .SB3(SB3), .SB4(SB4),
    .SB5(SB5), .SB6(SB6), .SB7(SB7), .nADDx(alu_add_1_naddx), .out0(alu_bcd_1_out0[0]),
    .out1(alu_bcd_1_out0[1]), .out2(alu_bcd_1_out0[2]), .out3(alu_bcd_1_out0[3]), .out4(alu_bcd_1_out0[4]),
    .out5(alu_bcd_1_out0[5]), .out6(alu_bcd_1_out0[6]), .out7(alu_bcd_1_out0[7]), .ncarry3(alu_ops_1_ncarry3));
  ALU_AC alu_ac_1 (
    .PHI2(PHI2), .SB_AC(SB_AC), .AC_SB(AC_SB), .AC_DB(AC_DB), .SB_DB(SB_DB), .SB_ADH(SB_ADH),
    .ins(alu_bcd_1_out0), .SB_In({SB7, SB6, SB5, SB4, SB3, SB2, SB1, SB0}),
    .SB_Out({SB7_2, SB6_2, SB5_2, SB4_2, SB3_2, SB2_2, SB1_2, SB0_2}),
    .DB_Out({DB7_2, DB6_2, DB5_2, DB4_2, DB3_2, DB2_2, DB1_2, DB0_2}),
    .ADH_Out({ADH7, ADH6, ADH5, ADH4, ADH3, ADH2, ADH1, ADH0}), .AC_Debug(AC_Debug),
    .DB_In({DB7, DB6, DB5, DB4, DB3, DB2, DB1, DB0}), .ADH_In(ADH_In), .SB_Dirty(SB_Dirty),
    .DB_Dirty(DB_Dirty), .ADH_Dirty(ADH_Dirty));

  // Notes on the sheet:
  //   x8
  //   AVR
  //   x8
  //   ACR
  //   x8
endmodule

module PC (
  input  PHI2,
  input  ADL_PCL,
  input  PCL_PCL,
  input  PCL_ADL,
  input  PCL_DB,
  input  ADH_PCH,
  input  PCH_PCH,
  input  PCH_ADH,
  input  PCH_DB,
  input  _1_PC,
  input  ADL0,
  input  ADL1,
  input  ADL2,
  input  ADL3,
  input  ADL4,
  input  ADL5,
  input  ADL6,
  input  ADL7,
  input  ADH0,
  input  ADH1,
  input  ADH2,
  input  ADH3,
  input  ADH4,
  input  ADH5,
  input  ADH6,
  input  ADH7,
  output DB0,
  output DB1,
  output DB2,
  output DB3,
  output DB4,
  output DB5,
  output DB6,
  output DB7,
  output ADL0_2,
  output ADL1_2,
  output ADL2_2,
  output ADL3_2,
  output ADL4_2,
  output ADL5_2,
  output ADL6_2,
  output ADL7_2,
  output ADH0_2,
  output ADH1_2,
  output ADH2_2,
  output ADH3_2,
  output ADH4_2,
  output ADH5_2,
  output ADH6_2,
  output ADH7_2,
  output [15:0] PC_Debug,
  output [15:0] PCS_Debug
);

  wire pcl_1_pclc;

  PCL pcl_1 (
    .PHI2(PHI2), .cin(_1_PC), .ADL_PCL(ADL_PCL), .PCL_PCL(PCL_PCL), .PCL_ADL(PCL_ADL), .PCL_DB(PCL_DB),
    .ADL0(ADL0), .ADL1(ADL1), .ADL2(ADL2), .ADL3(ADL3), .ADL4(ADL4), .ADL5(ADL5), .ADL6(ADL6), .ADL7(ADL7),
    .ADL0_2(ADL0_2), .ADL1_2(ADL1_2), .ADL2_2(ADL2_2), .ADL3_2(ADL3_2), .ADL4_2(ADL4_2), .ADL5_2(ADL5_2),
    .ADL6_2(ADL6_2), .ADL7_2(ADL7_2), .DB0(DB0), .DB1(DB1), .DB2(DB2), .DB3(DB3), .DB4(DB4), .DB5(DB5),
    .DB6(DB6), .DB7(DB7), .PCLC(pcl_1_pclc), .PCL_Debug(PC_Debug[7:0]), .PCLS_Debug(PCS_Debug[7:0]));
  PCH pch_1 (
    .PHI2(PHI2), .cin(pcl_1_pclc), .ADH_PCH(ADH_PCH), .PCH_PCH(PCH_PCH), .PCH_ADH(PCH_ADH), .PCH_DB(PCH_DB),
    .ADH0(ADH0), .ADH1(ADH1), .ADH2(ADH2), .ADH3(ADH3), .ADH4(ADH4), .ADH5(ADH5), .ADH6(ADH6), .ADH7(ADH7),
    .ADH0_2(ADH0_2), .ADH1_2(ADH1_2), .ADH2_2(ADH2_2), .ADH3_2(ADH3_2), .ADH4_2(ADH4_2), .ADH5_2(ADH5_2),
    .ADH6_2(ADH6_2), .ADH7_2(ADH7_2), .DB0(DB0), .DB1(DB1), .DB2(DB2), .DB3(DB3), .DB4(DB4), .DB5(DB5),
    .DB6(DB6), .DB7(DB7), .PCH_Debug(PC_Debug[15:8]), .PCHS_Debug(PCS_Debug[15:8]));
endmodule

module ABL_BIT (
  input  PHI1,
  input  PHI2,
  input  ADL_ABL,
  input  ADLx,
  output Ax
);

  wire and_1_out, not1_out;

  and and_1 (and_1_out, PHI1, ADL_ABL);
  not not1 (not1_out, ADLx);
  DFF_Level dff_level_1 (.EN(and_1_out), .D(not1_out), .NOT_Q(Ax));  // open: Q

  // Notes on the sheet:
  //   not used
endmodule

module ABH_BIT (
  input  PHI1,
  input  PHI2,
  input  ADH_ABH,
  input  ADHx,
  output Ax
);

  wire and_1_out, not1_out;

  and and_1 (and_1_out, PHI1, ADH_ABH);
  not not1 (not1_out, ADHx);
  DFF_Level dff_level_1 (.EN(and_1_out), .D(not1_out), .NOT_Q(Ax));  // open: Q

  // Notes on the sheet:
  //   not used
endmodule

module PCL_EVEN_BIT (
  input  PHI2,
  input  cin,
  input  ADL_PCL,
  input  PCL_PCL,
  input  PCL_ADL,
  input  PCL_DB,
  input  ADLx,
  output DBx,
  output ADLx_2,
  output cout,
  output sout,
  output PCL_Debug,
  output PCLS_Debug
);

  wire and_1_out, controlled_buffer_1_out, nand_1_out, not_1_out, PCL_not_q;

  nor nor_1 (cout, cin, sout);
  assign controlled_buffer_1_out = PCL_PCL ? PCL_Debug : 1'bz;  // Controlled_Buffer controlled_buffer_1
  assign controlled_buffer_1_out = ADL_PCL ? ADLx : 1'bz;  // Controlled_Buffer controlled_buffer_2
  nand nand_1 (nand_1_out, cin, sout);
  not not_1 (not_1_out, cout);
  DFF_Posedge PCL (.EN(PHI2), .D(and_1_out), .NOT_Q(PCL_not_q));  // open: Q
  DFF_Level PCLS (.EN(1'b1), .D(controlled_buffer_1_out), .Q(PCLS_Debug), .NOT_Q(sout));
  and and_1 (and_1_out, nand_1_out, not_1_out);
  not not_2 (PCL_Debug, PCL_not_q);
  assign DBx = PCL_DB ? PCL_Debug : 1'bz;  // Controlled_Buffer controlled_buffer_3
  assign ADLx_2 = PCL_ADL ? PCL_Debug : 1'bz;  // Controlled_Buffer controlled_buffer_4
endmodule

module PCL_ODD_BIT (
  input  PHI2,
  input  cin,
  input  ADL_PCL,
  input  PCL_PCL,
  input  PCL_ADL,
  input  PCL_DB,
  input  ADLx,
  output DBx,
  output ADLx_2,
  output cout,
  output sout,
  output PCL_Debug,
  output PCLS_Debug
);

  wire controlled_buffer_1_out, nor_1_out, not_1_out, not_2_out, not_3_out, or_1_out;

  not not_1 (not_1_out, sout);
  nand nand_1 (cout, cin, not_2_out);
  not not_2 (not_2_out, sout);
  nor nor_1 (nor_1_out, cin, not_1_out);
  not not_3 (not_3_out, cout);
  DFF_Posedge PCL (.EN(PHI2), .D(or_1_out), .NOT_Q(PCL_Debug));  // open: Q
  assign controlled_buffer_1_out = PCL_PCL ? PCL_Debug : 1'bz;  // Controlled_Buffer controlled_buffer_1
  assign controlled_buffer_1_out = ADL_PCL ? ADLx : 1'bz;  // Controlled_Buffer controlled_buffer_2
  DFF_Level PCLS (.EN(1'b1), .D(controlled_buffer_1_out), .Q(PCLS_Debug), .NOT_Q(sout));
  or or_1 (or_1_out, nor_1_out, not_3_out);
  assign DBx = PCL_DB ? PCL_Debug : 1'bz;  // Controlled_Buffer controlled_buffer_3
  assign ADLx_2 = PCL_ADL ? PCL_Debug : 1'bz;  // Controlled_Buffer controlled_buffer_4
endmodule

module PCH_EVEN_BIT (
  input  PHI2,
  input  cin,
  input  ADH_PCH,
  input  PCH_PCH,
  input  PCH_ADH,
  input  PCH_DB,
  input  ADHx,
  output DBx,
  output ADHx_2,
  output cout,
  output sout,
  output PCH_Debug,
  output PCHS_Debug
);

  wire controlled_buffer_1_out, nor_1_out, not_1_out, not_2_out, not_3_out, or_1_out;

  not not_1 (not_1_out, sout);
  nand nand_1 (cout, cin, not_2_out);
  not not_2 (not_2_out, sout);
  nor nor_1 (nor_1_out, cin, not_1_out);
  not not_3 (not_3_out, cout);
  DFF_Posedge PCH (.EN(PHI2), .D(or_1_out), .NOT_Q(PCH_Debug));  // open: Q
  assign controlled_buffer_1_out = PCH_PCH ? PCH_Debug : 1'bz;  // Controlled_Buffer controlled_buffer_1
  assign controlled_buffer_1_out = ADH_PCH ? ADHx : 1'bz;  // Controlled_Buffer controlled_buffer_2
  DFF_Level PCHS (.EN(1'b1), .D(controlled_buffer_1_out), .Q(PCHS_Debug), .NOT_Q(sout));
  or or_1 (or_1_out, nor_1_out, not_3_out);
  assign DBx = PCH_DB ? PCH_Debug : 1'bz;  // Controlled_Buffer controlled_buffer_3
  assign ADHx_2 = PCH_ADH ? PCH_Debug : 1'bz;  // Controlled_Buffer controlled_buffer_4
endmodule

module PCH_ODD_BIT (
  input  PHI2,
  input  cin,
  input  ADH_PCH,
  input  PCH_PCH,
  input  PCH_ADH,
  input  PCH_DB,
  input  ADHx,
  output DBx,
  output ADHx_2,
  output cout,
  output sout,
  output PCH_Debug,
  output PCHS_Debug
);

  wire and_1_out, controlled_buffer_1_out, nand_1_out, not_1_out, PCH_not_q;

  nor nor_1 (cout, cin, sout);
  assign controlled_buffer_1_out = PCH_PCH ? PCH_Debug : 1'bz;  // Controlled_Buffer controlled_buffer_1
  assign controlled_buffer_1_out = ADH_PCH ? ADHx : 1'bz;  // Controlled_Buffer controlled_buffer_2
  nand nand_1 (nand_1_out, cin, sout);
  not not_1 (not_1_out, cout);
  DFF_Posedge PCH (.EN(PHI2), .D(and_1_out), .NOT_Q(PCH_not_q));  // open: Q
  DFF_Level PCHS (.EN(1'b1), .D(controlled_buffer_1_out), .Q(PCHS_Debug), .NOT_Q(sout));
  and and_1 (and_1_out, nand_1_out, not_1_out);
  not not_2 (PCH_Debug, PCH_not_q);
  assign DBx = PCH_DB ? PCH_Debug : 1'bz;  // Controlled_Buffer controlled_buffer_3
  assign ADHx_2 = PCH_ADH ? PCH_Debug : 1'bz;  // Controlled_Buffer controlled_buffer_4
endmodule

module PCL (
  input  PHI2,
  input  cin,
  input  ADL_PCL,
  input  PCL_PCL,
  input  PCL_ADL,
  input  PCL_DB,
  input  ADL0,
  input  ADL1,
  input  ADL2,
  input  ADL3,
  input  ADL4,
  input  ADL5,
  input  ADL6,
  input  ADL7,
  output [7:0] PCL_Debug,
  output [7:0] PCLS_Debug,
  output ADL0_2,
  output ADL1_2,
  output ADL2_2,
  output ADL3_2,
  output ADL4_2,
  output ADL5_2,
  output ADL6_2,
  output ADL7_2,
  output DB0,
  output DB1,
  output DB2,
  output DB3,
  output DB4,
  output DB5,
  output DB6,
  output DB7,
  output PCLC
);

  wire _0_cout, _0_sout, _1_cout, _1_sout, _2_cout, _2_sout, _3_cout, _3_sout, _4_cout, _4_sout, _5_cout,
       _5_sout, _6_cout, _6_sout, _7_sout;

  PCL_EVEN_BIT _0 (
    .PHI2(PHI2), .cin(cin), .ADL_PCL(ADL_PCL), .PCL_PCL(PCL_PCL), .PCL_ADL(PCL_ADL), .PCL_DB(PCL_DB),
    .ADLx(ADL0), .ADLx_2(ADL0_2), .DBx(DB0), .cout(_0_cout), .PCL_Debug(PCL_Debug[0]),
    .PCLS_Debug(PCLS_Debug[0]), .sout(_0_sout));
  PCL_ODD_BIT _1 (
    .PHI2(PHI2), .cin(_0_cout), .ADL_PCL(ADL_PCL), .PCL_PCL(PCL_PCL), .PCL_ADL(PCL_ADL), .PCL_DB(PCL_DB),
    .ADLx(ADL1), .ADLx_2(ADL1_2), .DBx(DB1), .cout(_1_cout), .PCL_Debug(PCL_Debug[1]),
    .PCLS_Debug(PCLS_Debug[1]), .sout(_1_sout));
  PCL_EVEN_BIT _2 (
    .PHI2(PHI2), .cin(_1_cout), .ADL_PCL(ADL_PCL), .PCL_PCL(PCL_PCL), .PCL_ADL(PCL_ADL), .PCL_DB(PCL_DB),
    .ADLx(ADL2), .ADLx_2(ADL2_2), .DBx(DB2), .cout(_2_cout), .PCL_Debug(PCL_Debug[2]),
    .PCLS_Debug(PCLS_Debug[2]), .sout(_2_sout));
  PCL_ODD_BIT _3 (
    .PHI2(PHI2), .cin(_2_cout), .ADL_PCL(ADL_PCL), .PCL_PCL(PCL_PCL), .PCL_ADL(PCL_ADL), .PCL_DB(PCL_DB),
    .ADLx(ADL3), .ADLx_2(ADL3_2), .DBx(DB3), .cout(_3_cout), .PCL_Debug(PCL_Debug[3]),
    .PCLS_Debug(PCLS_Debug[3]), .sout(_3_sout));
  PCL_EVEN_BIT _4 (
    .PHI2(PHI2), .cin(_3_cout), .ADL_PCL(ADL_PCL), .PCL_PCL(PCL_PCL), .PCL_ADL(PCL_ADL), .PCL_DB(PCL_DB),
    .ADLx(ADL4), .ADLx_2(ADL4_2), .DBx(DB4), .cout(_4_cout), .PCL_Debug(PCL_Debug[4]),
    .PCLS_Debug(PCLS_Debug[4]), .sout(_4_sout));
  PCL_ODD_BIT _5 (
    .PHI2(PHI2), .cin(_4_cout), .ADL_PCL(ADL_PCL), .PCL_PCL(PCL_PCL), .PCL_ADL(PCL_ADL), .PCL_DB(PCL_DB),
    .ADLx(ADL5), .ADLx_2(ADL5_2), .DBx(DB5), .cout(_5_cout), .PCL_Debug(PCL_Debug[5]),
    .PCLS_Debug(PCLS_Debug[5]), .sout(_5_sout));
  PCL_EVEN_BIT _6 (
    .PHI2(PHI2), .cin(_5_cout), .ADL_PCL(ADL_PCL), .PCL_PCL(PCL_PCL), .PCL_ADL(PCL_ADL), .PCL_DB(PCL_DB),
    .ADLx(ADL6), .ADLx_2(ADL6_2), .DBx(DB6), .cout(_6_cout), .PCL_Debug(PCL_Debug[6]),
    .PCLS_Debug(PCLS_Debug[6]), .sout(_6_sout));
  PCL_ODD_BIT _7 (
    .PHI2(PHI2), .cin(_6_cout), .ADL_PCL(ADL_PCL), .PCL_PCL(PCL_PCL), .PCL_ADL(PCL_ADL), .PCL_DB(PCL_DB),
    .ADLx(ADL7), .ADLx_2(ADL7_2), .DBx(DB7), .PCL_Debug(PCL_Debug[7]), .PCLS_Debug(PCLS_Debug[7]),
    .sout(_7_sout));  // open: cout
  nor nor_1 (PCLC, _0_sout, _1_sout, _2_sout, _3_sout, cin, _4_sout, _5_sout, _6_sout, _7_sout);
endmodule

module PCH (
  input  PHI2,
  input  cin,
  input  ADH_PCH,
  input  PCH_PCH,
  input  PCH_ADH,
  input  PCH_DB,
  input  ADH0,
  input  ADH1,
  input  ADH2,
  input  ADH3,
  input  ADH4,
  input  ADH5,
  input  ADH6,
  input  ADH7,
  output ADH0_2,
  output ADH1_2,
  output ADH2_2,
  output ADH3_2,
  output ADH4_2,
  output ADH5_2,
  output ADH6_2,
  output ADH7_2,
  output DB0,
  output DB1,
  output DB2,
  output DB3,
  output DB4,
  output DB5,
  output DB6,
  output DB7,
  output [7:0] PCH_Debug,
  output [7:0] PCHS_Debug
);

  wire _0_cout, _0_sout, _1_cout, _1_sout, _2_cout, _2_sout, _3_sout, _4_cout, _5_cout, _6_cout, nor_1_out,
       not_1_out;

  not not_1 (not_1_out, cin);
  PCH_EVEN_BIT _0 (
    .PHI2(PHI2), .cin(cin), .ADH_PCH(ADH_PCH), .PCH_PCH(PCH_PCH), .PCH_ADH(PCH_ADH), .PCH_DB(PCH_DB),
    .ADHx(ADH0), .ADHx_2(ADH0_2), .DBx(DB0), .cout(_0_cout), .PCH_Debug(PCH_Debug[0]),
    .PCHS_Debug(PCHS_Debug[0]), .sout(_0_sout));
  PCH_ODD_BIT _1 (
    .PHI2(PHI2), .cin(_0_cout), .ADH_PCH(ADH_PCH), .PCH_PCH(PCH_PCH), .PCH_ADH(PCH_ADH), .PCH_DB(PCH_DB),
    .ADHx(ADH1), .ADHx_2(ADH1_2), .DBx(DB1), .cout(_1_cout), .PCH_Debug(PCH_Debug[1]),
    .PCHS_Debug(PCHS_Debug[1]), .sout(_1_sout));
  PCH_EVEN_BIT _2 (
    .PHI2(PHI2), .cin(_1_cout), .ADH_PCH(ADH_PCH), .PCH_PCH(PCH_PCH), .PCH_ADH(PCH_ADH), .PCH_DB(PCH_DB),
    .ADHx(ADH2), .ADHx_2(ADH2_2), .DBx(DB2), .cout(_2_cout), .PCH_Debug(PCH_Debug[2]),
    .PCHS_Debug(PCHS_Debug[2]), .sout(_2_sout));
  PCH_ODD_BIT _3 (
    .PHI2(PHI2), .cin(_2_cout), .ADH_PCH(ADH_PCH), .PCH_PCH(PCH_PCH), .PCH_ADH(PCH_ADH), .PCH_DB(PCH_DB),
    .ADHx(ADH3), .ADHx_2(ADH3_2), .DBx(DB3), .PCH_Debug(PCH_Debug[3]), .PCHS_Debug(PCHS_Debug[3]),
    .sout(_3_sout));  // open: cout
  PCH_EVEN_BIT _4 (
    .PHI2(PHI2), .cin(nor_1_out), .ADH_PCH(ADH_PCH), .PCH_PCH(PCH_PCH), .PCH_ADH(PCH_ADH), .PCH_DB(PCH_DB),
    .ADHx(ADH4), .ADHx_2(ADH4_2), .DBx(DB4), .cout(_4_cout), .PCH_Debug(PCH_Debug[4]),
    .PCHS_Debug(PCHS_Debug[4]));  // open: sout
  PCH_ODD_BIT _5 (
    .PHI2(PHI2), .cin(_4_cout), .ADH_PCH(ADH_PCH), .PCH_PCH(PCH_PCH), .PCH_ADH(PCH_ADH), .PCH_DB(PCH_DB),
    .ADHx(ADH5), .ADHx_2(ADH5_2), .DBx(DB5), .cout(_5_cout), .PCH_Debug(PCH_Debug[5]),
    .PCHS_Debug(PCHS_Debug[5]));  // open: sout
  PCH_EVEN_BIT _6 (
    .PHI2(PHI2), .cin(_5_cout), .ADH_PCH(ADH_PCH), .PCH_PCH(PCH_PCH), .PCH_ADH(PCH_ADH), .PCH_DB(PCH_DB),
    .ADHx(ADH6), .ADHx_2(ADH6_2), .DBx(DB6), .cout(_6_cout), .PCH_Debug(PCH_Debug[6]),
    .PCHS_Debug(PCHS_Debug[6]));  // open: sout
  PCH_ODD_BIT _7 (
    .PHI2(PHI2), .cin(_6_cout), .ADH_PCH(ADH_PCH), .PCH_PCH(PCH_PCH), .PCH_ADH(PCH_ADH), .PCH_DB(PCH_DB),
    .ADHx(ADH7), .ADHx_2(ADH7_2), .DBx(DB7), .PCH_Debug(PCH_Debug[7]), .PCHS_Debug(PCHS_Debug[7]));  // open: cout, sout
  nor nor_1 (nor_1_out, not_1_out, _0_sout, _1_sout, _2_sout, _3_sout);

  // Notes on the sheet:
  //   PCHC
endmodule

module ALU_OPS (
  input  NDB_ADD,
  input  DB_ADD,
  input  _0_ADD,
  input  SB_ADD,
  input  ADL_ADD,
  input  ANDS,
  input  EORS,
  input  ORS,
  input  SRS,
  input  SUMS,
  input  ncin,
  input  DC3,
  input  SB0,
  input  SB1,
  input  SB2,
  input  SB3,
  input  SB4,
  input  SB5,
  input  SB6,
  input  SB7,
  input  DB0,
  input  DB1,
  input  DB2,
  input  DB3,
  input  DB4,
  input  DB5,
  input  DB6,
  input  DB7,
  input  ADL0,
  input  ADL1,
  input  ADL2,
  input  ADL3,
  input  ADL4,
  input  ADL5,
  input  ADL6,
  input  ADL7,
  output ncarry3,
  output carry4,
  output carry6,
  output ncarry7,
  output res0,
  output res1,
  output res2,
  output res3,
  output res4,
  output res5,
  output res6,
  output res7,
  output nor0,
  output nor1,
  output nor2,
  output nor3,
  output nor4,
  output nor5,
  output nor6,
  output nor7,
  output nand0,
  output nand1,
  output nand2,
  output nand3,
  output nand4,
  output nand5,
  output nand6,
  output nand7,
  output xor0,
  output xor1,
  output xor2,
  output xor3,
  output xor4,
  output xor5,
  output xor6,
  output xor7,
  output [7:0] AI_Debug,
  output [7:0] BI_Debug
);

  wire _0_cout, _1_ncout, _2_cout, _5_ncout, and_1_out, not_1_out;

  ALU_EVEN_BIT _0 (
    .NDB_ADD(NDB_ADD), .DB_ADD(DB_ADD), ._0_ADD(_0_ADD), .SB_ADD(SB_ADD), .ADL_ADD(ADL_ADD), .ANDS(ANDS),
    .EORS(EORS), .ORS(ORS), .SRS(SRS), .SUMS(SUMS), .ncin(ncin), .prev_res(nand1), .SBx(SB0), .DBx(DB0),
    .ADLx(ADL0), .nres(res0), .cout(_0_cout), .\nor (nor0), .\nand (nand0), .\xor (xor0),
    .AI_Debug(AI_Debug[0]), .BI_Debug(BI_Debug[0]));
  ALU_ODD_BIT _1 (
    .NDB_ADD(NDB_ADD), .DB_ADD(DB_ADD), ._0_ADD(_0_ADD), .SB_ADD(SB_ADD), .ADL_ADD(ADL_ADD), .ANDS(ANDS),
    .EORS(EORS), .ORS(ORS), .SRS(SRS), .SUMS(SUMS), .cin(_0_cout), .prev_res(nand2), .SBx(SB1), .DBx(DB1),
    .ADLx(ADL1), .nres(res1), .ncout(_1_ncout), .\nor (nor1), .\nand (nand1), .\xor (xor1),
    .AI_Debug(AI_Debug[1]), .BI_Debug(BI_Debug[1]));
  ALU_EVEN_BIT _2 (
    .NDB_ADD(NDB_ADD), .DB_ADD(DB_ADD), ._0_ADD(_0_ADD), .SB_ADD(SB_ADD), .ADL_ADD(ADL_ADD), .ANDS(ANDS),
    .EORS(EORS), .ORS(ORS), .SRS(SRS), .SUMS(SUMS), .ncin(_1_ncout), .prev_res(nand3), .SBx(SB2), .DBx(DB2),
    .ADLx(ADL2), .nres(res2), .cout(_2_cout), .\nor (nor2), .\nand (nand2), .\xor (xor2),
    .AI_Debug(AI_Debug[2]), .BI_Debug(BI_Debug[2]));
  ALU_ODD_BIT _3 (
    .NDB_ADD(NDB_ADD), .DB_ADD(DB_ADD), ._0_ADD(_0_ADD), .SB_ADD(SB_ADD), .ADL_ADD(ADL_ADD), .ANDS(ANDS),
    .EORS(EORS), .ORS(ORS), .SRS(SRS), .SUMS(SUMS), .cin(_2_cout), .prev_res(nand4), .SBx(SB3), .DBx(DB3),
    .ADLx(ADL3), .nres(res3), .ncout(ncarry3), .\nor (nor3), .\nand (nand3), .\xor (xor3),
    .AI_Debug(AI_Debug[3]), .BI_Debug(BI_Debug[3]));
  not not_1 (not_1_out, DC3);
  and and_1 (and_1_out, ncarry3, not_1_out);
  ALU_EVEN_BIT _4 (
    .NDB_ADD(NDB_ADD), .DB_ADD(DB_ADD), ._0_ADD(_0_ADD), .SB_ADD(SB_ADD), .ADL_ADD(ADL_ADD), .ANDS(ANDS),
    .EORS(EORS), .ORS(ORS), .SRS(SRS), .SUMS(SUMS), .ncin(and_1_out), .prev_res(nand5), .SBx(SB4), .DBx(DB4),
    .ADLx(ADL4), .nres(res4), .cout(carry4), .\nor (nor4), .\nand (nand4), .\xor (xor4),
    .AI_Debug(AI_Debug[4]), .BI_Debug(BI_Debug[4]));
  ALU_ODD_BIT _5 (
    .NDB_ADD(NDB_ADD), .DB_ADD(DB_ADD), ._0_ADD(_0_ADD), .SB_ADD(SB_ADD), .ADL_ADD(ADL_ADD), .ANDS(ANDS),
    .EORS(EORS), .ORS(ORS), .SRS(SRS), .SUMS(SUMS), .cin(carry4), .prev_res(nand6), .SBx(SB5), .DBx(DB5),
    .ADLx(ADL5), .nres(res5), .ncout(_5_ncout), .\nor (nor5), .\nand (nand5), .\xor (xor5),
    .AI_Debug(AI_Debug[5]), .BI_Debug(BI_Debug[5]));
  ALU_EVEN_BIT _6 (
    .NDB_ADD(NDB_ADD), .DB_ADD(DB_ADD), ._0_ADD(_0_ADD), .SB_ADD(SB_ADD), .ADL_ADD(ADL_ADD), .ANDS(ANDS),
    .EORS(EORS), .ORS(ORS), .SRS(SRS), .SUMS(SUMS), .ncin(_5_ncout), .prev_res(nand7), .SBx(SB6), .DBx(DB6),
    .ADLx(ADL6), .nres(res6), .cout(carry6), .\nor (nor6), .\nand (nand6), .\xor (xor6),
    .AI_Debug(AI_Debug[6]), .BI_Debug(BI_Debug[6]));
  ALU_ODD_BIT _7 (
    .NDB_ADD(NDB_ADD), .DB_ADD(DB_ADD), ._0_ADD(_0_ADD), .SB_ADD(SB_ADD), .ADL_ADD(ADL_ADD), .ANDS(ANDS),
    .EORS(EORS), .ORS(ORS), .SRS(SRS), .SUMS(SUMS), .cin(carry6), .prev_res(1'b1), .SBx(SB7), .DBx(DB7),
    .ADLx(ADL7), .nres(res7), .ncout(ncarry7), .\nor (nor7), .\nand (nand7), .\xor (xor7),
    .AI_Debug(AI_Debug[7]), .BI_Debug(BI_Debug[7]));
endmodule

module ALU_EVEN_BIT (
  input  NDB_ADD,
  input  DB_ADD,
  input  _0_ADD,
  input  SB_ADD,
  input  ADL_ADD,
  input  ANDS,
  input  EORS,
  input  ORS,
  input  SRS,
  input  SUMS,
  input  ncin,
  input  prev_res,
  input  SBx,
  input  DBx,
  input  ADLx,
  output nres,
  output cout,
  output AI_Debug,
  output \nor ,
  output \nand ,
  output BI_Debug,
  output \xor 
);

  wire and_1_out, controlled_buffer_1_out, controlled_buffer_3_out, nand_2_out, nand_3_out, nand_4_out,
       nor_2_out, not_1_out, not_2_out, not_3_out, not_4_out, not_5_out;

  assign controlled_buffer_1_out = _0_ADD ? 1'b0 : 1'bz;  // Controlled_Buffer controlled_buffer_1
  assign controlled_buffer_1_out = SB_ADD ? SBx : 1'bz;  // Controlled_Buffer controlled_buffer_2
  assign controlled_buffer_3_out = DB_ADD ? DBx : 1'bz;  // Controlled_Buffer controlled_buffer_3
  assign controlled_buffer_3_out = NDB_ADD ? not_1_out : 1'bz;  // Controlled_Buffer controlled_buffer_4
  not not_1 (not_1_out, DBx);
  assign controlled_buffer_3_out = ADL_ADD ? ADLx : 1'bz;  // Controlled_Buffer controlled_buffer_5
  not not_2 (not_2_out, \nor );
  not not_3 (not_3_out, ncin);
  D_Latch AI (.EN(1'b1), .D(controlled_buffer_1_out), .Q(AI_Debug));  // open: NOT_Q
  D_Latch BI (.EN(1'b1), .D(controlled_buffer_3_out), .Q(BI_Debug));  // open: NOT_Q
  nand nand_1 (\nand , AI_Debug, BI_Debug);
  nor nor_1 (\nor , AI_Debug, BI_Debug);
  nand nand_2 (nand_2_out, not_2_out, \nand );
  nand nand_3 (nand_3_out, not_3_out, nand_2_out);
  not not_4 (not_4_out, nor_2_out);
  nor nor_2 (nor_2_out, not_3_out, nand_2_out);
  nand nand_4 (nand_4_out, ncin, \nand );
  not not_5 (not_5_out, \nor );
  and and_1 (and_1_out, nand_3_out, not_4_out);
  and and_2 (cout, nand_4_out, not_5_out);
  assign nres = ANDS ? \nand  : 1'bz;  // Controlled_Buffer controlled_buffer_6
  assign nres = ORS ? \nor  : 1'bz;  // Controlled_Buffer controlled_buffer_7
  assign nres = EORS ? nand_2_out : 1'bz;  // Controlled_Buffer controlled_buffer_8
  assign nres = SRS ? prev_res : 1'bz;  // Controlled_Buffer controlled_buffer_9
  assign nres = SUMS ? and_1_out : 1'bz;  // Controlled_Buffer controlled_buffer_10
  not not_6 (\xor , nand_2_out);

  // Notes on the sheet:
  //   xnor
  //   xor
endmodule

module ALU_ODD_BIT (
  input  NDB_ADD,
  input  DB_ADD,
  input  _0_ADD,
  input  SB_ADD,
  input  ADL_ADD,
  input  ANDS,
  input  EORS,
  input  ORS,
  input  SRS,
  input  SUMS,
  input  cin,
  input  prev_res,
  input  SBx,
  input  DBx,
  input  ADLx,
  output nres,
  output ncout,
  output AI_Debug,
  output \nor ,
  output \nand ,
  output BI_Debug,
  output \xor 
);

  wire and_1_out, controlled_buffer_1_out, controlled_buffer_3_out, nand_2_out, nand_3_out, nor_3_out,
       not_1_out, not_2_out, not_3_out, not_4_out, not_5_out, not_6_out;

  assign controlled_buffer_1_out = _0_ADD ? 1'b0 : 1'bz;  // Controlled_Buffer controlled_buffer_1
  assign controlled_buffer_1_out = SB_ADD ? SBx : 1'bz;  // Controlled_Buffer controlled_buffer_2
  assign controlled_buffer_3_out = DB_ADD ? DBx : 1'bz;  // Controlled_Buffer controlled_buffer_3
  not not_1 (not_1_out, DBx);
  assign controlled_buffer_3_out = NDB_ADD ? not_1_out : 1'bz;  // Controlled_Buffer controlled_buffer_4
  assign controlled_buffer_3_out = ADL_ADD ? ADLx : 1'bz;  // Controlled_Buffer controlled_buffer_5
  not not_2 (not_2_out, \nand );
  not not_3 (not_3_out, cin);
  not not_4 (not_4_out, \nor );
  D_Latch AI (.EN(1'b1), .D(controlled_buffer_1_out), .Q(AI_Debug));  // open: NOT_Q
  D_Latch BI (.EN(1'b1), .D(controlled_buffer_3_out), .Q(BI_Debug));  // open: NOT_Q
  nand nand_1 (\nand , AI_Debug, BI_Debug);
  nor nor_1 (\nor , AI_Debug, BI_Debug);
  nor nor_2 (\xor , not_2_out, \nor );
  nand nand_2 (nand_2_out, not_3_out, \xor );
  not not_5 (not_5_out, nor_3_out);
  nor nor_3 (nor_3_out, not_3_out, \xor );
  nand nand_3 (nand_3_out, cin, not_4_out);
  not not_6 (not_6_out, not_2_out);
  and and_1 (and_1_out, nand_2_out, not_5_out);
  and and_2 (ncout, nand_3_out, not_6_out);
  assign nres = ANDS ? \nand  : 1'bz;  // Controlled_Buffer controlled_buffer_6
  assign nres = ORS ? \nor  : 1'bz;  // Controlled_Buffer controlled_buffer_7
  assign nres = EORS ? \xor  : 1'bz;  // Controlled_Buffer controlled_buffer_8
  assign nres = SRS ? prev_res : 1'bz;  // Controlled_Buffer controlled_buffer_9
  assign nres = SUMS ? and_1_out : 1'bz;  // Controlled_Buffer controlled_buffer_10

  // Notes on the sheet:
  //   xor
  //   xor
endmodule

module BCD_CARRY (
  input  nACIN,
  input  carry4,
  input  nDAA,
  input  [7:0] \nor ,
  input  [7:0] \nand ,
  input  [7:0] \xor ,
  output DC3,
  output DC7
);

  wire and_1_out, nand_1_out, nand_2_out, nand_3_out, nor_1_out, nor_2_out, nor_3_out, nor_4_out, nor_5_out,
       nor_6_out, nor_7_out, nor_8_out, nor_9_out, not_1_out, not_2_out, not_3_out, not_4_out, not_5_out,
       not_6_out, not_7_out, not_8_out, not_9_out, or_1_out, or_2_out;

  nand nand_1 (nand_1_out, nACIN, \nand [0]);
  not not_1 (not_1_out, \nor [0]);
  not not_2 (not_2_out, \nand [5]);
  not not_3 (not_3_out, \nand [2]);
  not not_4 (not_4_out, \nand [1]);
  and and_1 (and_1_out, nand_1_out, not_1_out);
  nor nor_1 (nor_1_out, not_3_out, \nor [2]);
  not not_5 (not_5_out, \nand [6]);
  nor nor_2 (nor_2_out, not_3_out, \xor [3]);
  nor nor_3 (nor_3_out, and_1_out, nor_1_out, not_4_out, \xor [1]);
  not not_6 (not_6_out, \nand [1]);
  nand nand_2 (nand_2_out, not_6_out, and_1_out);
  nor nor_4 (nor_4_out, \xor [7], not_5_out);
  nor nor_5 (nor_5_out, carry4, not_2_out, \xor [5], \xor [6]);
  not not_7 (not_7_out, \xor [6]);
  nand nand_3 (nand_3_out, not_2_out, carry4);
  nor nor_6 (nor_6_out, nor_2_out, nor_3_out);
  nor nor_7 (nor_7_out, \nor [2], nand_2_out);
  nor nor_8 (nor_8_out, nor_4_out, nor_5_out);
  nor nor_9 (nor_9_out, not_7_out, nand_3_out);
  or or_1 (or_1_out, nor_6_out, nor_7_out);
  not not_8 (not_8_out, nDAA);
  or or_2 (or_2_out, nor_8_out, nor_9_out);
  not not_9 (not_9_out, nDAA);
  and and_2 (DC3, or_1_out, not_8_out);
  and and_3 (DC7, or_2_out, not_9_out);

  // Notes on the sheet:
  //   b
  //   c
  //   ~(b | c)
  //   a
endmodule

module ALU_ADD (
  input  PHI2,
  input  ADD_SB06,
  input  ADD_SB7,
  input  ADD_ADL,
  input  [7:0] nres,
  output [7:0] nADDx,
  output SB0,
  output SB1,
  output SB2,
  output SB3,
  output SB4,
  output SB5,
  output SB6,
  output SB7,
  output ADL0,
  output ADL1,
  output ADL2,
  output ADL3,
  output ADL4,
  output ADL5,
  output ADL6,
  output ADL7,
  output [7:0] ADD_Debug
);

  D_Latch d_latch_1 (.EN(PHI2), .D(nres[0]), .Q(nADDx[0]), .NOT_Q(ADD_Debug[0]));
  D_Latch d_latch_2 (.EN(PHI2), .D(nres[1]), .Q(nADDx[1]), .NOT_Q(ADD_Debug[1]));
  D_Latch d_latch_3 (.EN(PHI2), .D(nres[2]), .Q(nADDx[2]), .NOT_Q(ADD_Debug[2]));
  D_Latch d_latch_4 (.EN(PHI2), .D(nres[3]), .Q(nADDx[3]), .NOT_Q(ADD_Debug[3]));
  D_Latch d_latch_5 (.EN(PHI2), .D(nres[4]), .Q(nADDx[4]), .NOT_Q(ADD_Debug[4]));
  D_Latch d_latch_6 (.EN(PHI2), .D(nres[5]), .Q(nADDx[5]), .NOT_Q(ADD_Debug[5]));
  D_Latch d_latch_7 (.EN(PHI2), .D(nres[6]), .Q(nADDx[6]), .NOT_Q(ADD_Debug[6]));
  D_Latch d_latch_8 (.EN(PHI2), .D(nres[7]), .Q(nADDx[7]), .NOT_Q(ADD_Debug[7]));
  assign SB0 = ADD_SB06 ? ADD_Debug[0] : 1'bz;  // Controlled_Buffer controlled_buffer_1
  assign SB1 = ADD_SB06 ? ADD_Debug[1] : 1'bz;  // Controlled_Buffer controlled_buffer_2
  assign SB2 = ADD_SB06 ? ADD_Debug[2] : 1'bz;  // Controlled_Buffer controlled_buffer_3
  assign SB3 = ADD_SB06 ? ADD_Debug[3] : 1'bz;  // Controlled_Buffer controlled_buffer_4
  assign SB4 = ADD_SB06 ? ADD_Debug[4] : 1'bz;  // Controlled_Buffer controlled_buffer_5
  assign SB5 = ADD_SB06 ? ADD_Debug[5] : 1'bz;  // Controlled_Buffer controlled_buffer_6
  assign SB6 = ADD_SB06 ? ADD_Debug[6] : 1'bz;  // Controlled_Buffer controlled_buffer_7
  assign SB7 = ADD_SB7 ? ADD_Debug[7] : 1'bz;  // Controlled_Buffer controlled_buffer_8
  assign ADL0 = ADD_ADL ? ADD_Debug[0] : 1'bz;  // Controlled_Buffer controlled_buffer_9
  assign ADL1 = ADD_ADL ? ADD_Debug[1] : 1'bz;  // Controlled_Buffer controlled_buffer_10
  assign ADL2 = ADD_ADL ? ADD_Debug[2] : 1'bz;  // Controlled_Buffer controlled_buffer_11
  assign ADL3 = ADD_ADL ? ADD_Debug[3] : 1'bz;  // Controlled_Buffer controlled_buffer_12
  assign ADL4 = ADD_ADL ? ADD_Debug[4] : 1'bz;  // Controlled_Buffer controlled_buffer_13
  assign ADL5 = ADD_ADL ? ADD_Debug[5] : 1'bz;  // Controlled_Buffer controlled_buffer_14
  assign ADL6 = ADD_ADL ? ADD_Debug[6] : 1'bz;  // Controlled_Buffer controlled_buffer_15
  assign ADL7 = ADD_ADL ? ADD_Debug[7] : 1'bz;  // Controlled_Buffer controlled_buffer_16
endmodule

module ALU_BCD (
  input  PHI2,
  input  ncarry3,
  input  ACR,
  input  nDAA,
  input  nDSA,
  input  SB0,
  input  SB1,
  input  SB2,
  input  SB3,
  input  SB4,
  input  SB5,
  input  SB6,
  input  SB7,
  input  [7:0] nADDx,
  output out0,
  output out1,
  output out2,
  output out3,
  output out4,
  output out5,
  output out6,
  output out7
);

  wire and_1_out, and_2_out, and_3_out, and_4_out, daah_latch_not_q, daal_latch_not_q, dsah_latch_not_q,
       dsal_latch_q, nand_1_out, nand_2_out, nand_3_out, nand_4_out, nand_5_out, nand_6_out, nand_7_out,
       nand_8_out, nand_9_out, nand_10_out, nand_11_out, nor_1_out, nor_2_out, nor_3_out, nor_4_out,
       nor_5_out, nor_6_out, nor_7_out, not_1_out, not_2_out, not_3_out, not_4_out, not_5_out, not_6_out,
       not_7_out, not_8_out, not_9_out, not_10_out, not_11_out, not_12_out;

  not not_1 (not_1_out, ncarry3);
  not not_2 (not_2_out, nDAA);
  nor nor_1 (nor_1_out, nADDx[1], nADDx[2]);
  not not_3 (not_3_out, nor_1_out);
  nand nand_1 (nand_1_out, nADDx[1], nADDx[2]);
  nand nand_2 (nand_2_out, nADDx[5], nADDx[6]);
  nor nor_2 (nor_2_out, nADDx[5], nADDx[6]);
  nand nand_3 (nand_3_out, not_2_out, not_1_out);
  nor nor_3 (nor_3_out, not_1_out, nDSA);
  not not_4 (not_4_out, nDSA);
  not not_5 (not_5_out, nor_2_out);
  D_Latch daal_latch (.EN(PHI2), .D(nand_3_out), .NOT_Q(daal_latch_not_q));  // open: Q
  not not_6 (not_6_out, ACR);
  D_Latch daah_latch (.EN(PHI2), .D(not_2_out), .NOT_Q(daah_latch_not_q));  // open: Q
  D_Latch dsal_latch (.EN(PHI2), .D(nor_3_out), .Q(dsal_latch_q));  // open: NOT_Q
  D_Latch dsah_latch (.EN(PHI2), .D(not_4_out), .NOT_Q(dsah_latch_not_q));  // open: Q
  nand nand_4 (nand_4_out, nADDx[1], daal_latch_not_q);
  and and_1 (and_1_out, nand_4_out, nand_5_out);
  nand nand_5 (nand_5_out, ~nADDx[1], dsal_latch_q);  // NAND_Gate
  nand nand_6 (nand_6_out, not_3_out, dsal_latch_q);
  and and_2 (and_2_out, nand_6_out, nand_7_out);
  nand nand_7 (nand_7_out, nand_1_out, daal_latch_not_q);
  nand nand_8 (nand_8_out, nADDx[5], nor_4_out);
  and and_3 (and_3_out, nand_8_out, nand_9_out);
  nand nand_9 (nand_9_out, ~nADDx[5], nor_5_out);  // NAND_Gate
  nand nand_10 (nand_10_out, nand_2_out, nor_4_out);
  and and_4 (and_4_out, nand_10_out, nand_11_out);
  nand nand_11 (nand_11_out, not_5_out, nor_5_out);
  nor nor_4 (nor_4_out, not_6_out, daah_latch_not_q);
  nor nor_5 (nor_5_out, ACR, dsah_latch_not_q);
  nor nor_6 (nor_6_out, dsal_latch_q, daal_latch_not_q);
  not not_7 (not_7_out, SB1);
  not not_8 (not_8_out, SB2);
  not not_9 (not_9_out, SB3);
  nor nor_7 (nor_7_out, nor_4_out, nor_5_out);
  not not_10 (not_10_out, SB5);
  not not_11 (not_11_out, SB6);
  not not_12 (not_12_out, SB7);
  xor xor_1 (out1, nor_6_out, not_7_out);
  xor xor_2 (out2, and_1_out, not_8_out);
  xor xor_3 (out3, and_2_out, not_9_out);
  xor xor_4 (out5, nor_7_out, not_10_out);
  xor xor_5 (out6, and_3_out, not_11_out);
  xor xor_6 (out7, and_4_out, not_12_out);

  assign out0 = SB0;
  assign out4 = SB4;

  // Notes on the sheet:
  //   DAAL
  //   DAAL
  //   DAAH
  //   DSAL
  //   DSAH
  //   DSAL
  //   DAAH
  //   DSAH
endmodule

module ALU_AC (
  input  PHI2,
  input  SB_AC,
  input  AC_SB,
  input  AC_DB,
  input  SB_DB,
  input  SB_ADH,
  input  [7:0] SB_In,
  input  [7:0] DB_In,
  input  [7:0] ins,
  input  [7:0] ADH_In,
  input  SB_Dirty,
  input  DB_Dirty,
  input  ADH_Dirty,
  output [7:0] AC_Debug,
  output [7:0] SB_Out,
  output [7:0] DB_Out,
  output [7:0] ADH_Out
);

  wire and_1_out, and_2_out, and_3_out, and_4_out, controlled_buffer_1_out, controlled_buffer_2_out,
       controlled_buffer_3_out, controlled_buffer_4_out, controlled_buffer_5_out, controlled_buffer_6_out,
       controlled_buffer_7_out, controlled_buffer_8_out;

  D_Latch d_latch_1 (.EN(PHI2), .D(controlled_buffer_1_out), .Q(AC_Debug[0]));  // open: NOT_Q
  assign controlled_buffer_1_out = SB_AC ? ins[0] : 1'bz;  // Controlled_Buffer controlled_buffer_1
  D_Latch d_latch_2 (.EN(PHI2), .D(controlled_buffer_2_out), .Q(AC_Debug[1]));  // open: NOT_Q
  assign controlled_buffer_2_out = SB_AC ? ins[1] : 1'bz;  // Controlled_Buffer controlled_buffer_2
  D_Latch d_latch_3 (.EN(PHI2), .D(controlled_buffer_3_out), .Q(AC_Debug[2]));  // open: NOT_Q
  assign controlled_buffer_3_out = SB_AC ? ins[2] : 1'bz;  // Controlled_Buffer controlled_buffer_3
  D_Latch d_latch_4 (.EN(PHI2), .D(controlled_buffer_4_out), .Q(AC_Debug[3]));  // open: NOT_Q
  assign controlled_buffer_4_out = SB_AC ? ins[3] : 1'bz;  // Controlled_Buffer controlled_buffer_4
  D_Latch d_latch_5 (.EN(PHI2), .D(controlled_buffer_5_out), .Q(AC_Debug[4]));  // open: NOT_Q
  assign controlled_buffer_5_out = SB_AC ? ins[4] : 1'bz;  // Controlled_Buffer controlled_buffer_5
  D_Latch d_latch_6 (.EN(PHI2), .D(controlled_buffer_6_out), .Q(AC_Debug[5]));  // open: NOT_Q
  assign controlled_buffer_6_out = SB_AC ? ins[5] : 1'bz;  // Controlled_Buffer controlled_buffer_6
  D_Latch d_latch_7 (.EN(PHI2), .D(controlled_buffer_7_out), .Q(AC_Debug[6]));  // open: NOT_Q
  assign controlled_buffer_7_out = SB_AC ? ins[6] : 1'bz;  // Controlled_Buffer controlled_buffer_7
  D_Latch d_latch_8 (.EN(PHI2), .D(controlled_buffer_8_out), .Q(AC_Debug[7]));  // open: NOT_Q
  assign controlled_buffer_8_out = SB_AC ? ins[7] : 1'bz;  // Controlled_Buffer controlled_buffer_8
  assign SB_Out = AC_SB ? AC_Debug : 8'bz;  // Controlled_Buffer controlled_buffer_9
  assign DB_Out = AC_DB ? AC_Debug : 8'bz;  // Controlled_Buffer controlled_buffer_10
  and and_1 (and_1_out, SB_DB, DB_Dirty);
  assign SB_Out = and_1_out ? DB_In : 8'bz;  // Controlled_Buffer controlled_buffer_11
  and and_2 (and_2_out, SB_ADH, SB_Dirty);
  assign ADH_Out = and_2_out ? SB_In : 8'bz;  // Controlled_Buffer controlled_buffer_12
  and and_3 (and_3_out, SB_DB, SB_Dirty);
  assign DB_Out = and_3_out ? SB_In : 8'bz;  // Controlled_Buffer controlled_buffer_13
  and and_4 (and_4_out, SB_ADH, ADH_Dirty);
  assign SB_Out = and_4_out ? ADH_In : 8'bz;  // Controlled_Buffer controlled_buffer_14
endmodule

module ADD_SB7 (
  input  PHI1,
  input  PHI2,
  input  nC_OUT,
  input  nready,
  input  SR,
  input  nROR,
  output nADD_SB7
);

  wire cout_latch_not_q, ff_latch1_not_q, ff_latch2_q, multiplexer_1_out, mux_latch1_q, nor_1_out, not_1_out,
       not_2_out, not_3_out, nready_latch_q, sr_latch1_not_q, sr_latch2_q;

  not not_1 (not_1_out, nC_OUT);
  D_Latch cout_latch (.EN(PHI2), .D(not_1_out), .NOT_Q(cout_latch_not_q));  // open: Q
  D_Latch nready_latch (.EN(PHI1), .D(nready), .Q(nready_latch_q));  // open: NOT_Q
  not not_2 (not_2_out, SR);
  nor nor_1 (nor_1_out, nready_latch_q, not_2_out);
  D_Latch mux_latch1 (.EN(PHI2), .D(nor_1_out), .Q(mux_latch1_q));  // open: NOT_Q
  D_Latch sr_latch1 (.EN(PHI2), .D(SR), .NOT_Q(sr_latch1_not_q));  // open: Q
  D_Latch ff_latch2 (.EN(PHI2), .D(ff_latch1_not_q), .Q(ff_latch2_q));  // open: NOT_Q
  not not_3 (not_3_out, multiplexer_1_out);
  Multiplexer #(.enable("false")) multiplexer_1 (
    .in0(ff_latch2_q), .in1(cout_latch_not_q), .out(multiplexer_1_out), .sel(mux_latch1_q));
  D_Latch ff_latch1 (.EN(PHI1), .D(not_3_out), .NOT_Q(ff_latch1_not_q));  // open: Q
  D_Latch sr_latch2 (.EN(PHI1), .D(sr_latch1_not_q), .Q(sr_latch2_q));  // open: NOT_Q
  nor nor_2 (nADD_SB7, ff_latch1_not_q, sr_latch2_q, nROR);

  // Notes on the sheet:
  //   FF
endmodule

module PRECHARGE (
  input  PHI2,
  input  _0_ADD,
  input  SB_ADD,
  input  [7:0] SB_In,
  input  [7:0] DB_In,
  input  [7:0] ADL_In,
  input  [7:0] ADH_In,
  output [7:0] SB_Out,
  output [7:0] DB_Out,
  output [7:0] ADL_Out,
  output [7:0] ADH_Out
);

  wire and_1_out, not_1_out;

  not not_1 (not_1_out, PHI2);
  and and_1 (and_1_out, not_1_out, _0_ADD, SB_ADD);
  Multiplexer #(.width(8)) multiplexer_1 (.in0(SB_In), .in1({8{1'b0}}), .out(SB_Out), .sel(and_1_out));  // open: en
  Multiplexer #(.width(8)) multiplexer_2 (.in0(DB_In), .in1({8{1'b0}}), .out(DB_Out), .sel(and_1_out));  // open: en
  Multiplexer #(.width(8)) multiplexer_3 (.in0(ADL_In), .in1({8{1'b0}}), .out(ADL_Out), .sel(and_1_out));  // open: en
  Multiplexer #(.width(8)) multiplexer_4 (.in0(ADH_In), .in1({8{1'b0}}), .out(ADH_Out), .sel(and_1_out));  // open: en

  // Notes on the sheet:
  //   ADH_In: pull=up
  //   DB_In: pull=up
  //   SB_In: pull=up
  //   ADL_In: pull=up
  //   Take into account that the tristate bus inputs are pulled up to 1, to simulate precharge.
endmodule

module CONST_GEN (
  input  _0_ADL0,
  input  _0_ADL1,
  input  _0_ADL2,
  input  [7:0] ADL_In,
  input  _0_ADH0,
  input  _0_ADH17,
  input  [7:0] ADH_In,
  output [7:0] ADL_Out,
  output [7:0] ADH_Out
);

  and and_1 (ADL_Out[0], ADL_In[0], ~_0_ADL0);  // AND_Gate
  and and_2 (ADL_Out[1], ADL_In[1], ~_0_ADL1);  // AND_Gate
  and and_3 (ADL_Out[2], ADL_In[2], ~_0_ADL2);  // AND_Gate
  and and_4 (ADH_Out[0], ADH_In[0], ~_0_ADH0);  // AND_Gate
  and and_5 (ADH_Out[1], ADH_In[1], ~_0_ADH17);  // AND_Gate
  and and_6 (ADH_Out[2], ADH_In[2], ~_0_ADH17);  // AND_Gate
  and and_7 (ADH_Out[3], ADH_In[3], ~_0_ADH17);  // AND_Gate
  and and_8 (ADH_Out[4], ADH_In[4], ~_0_ADH17);  // AND_Gate
  and and_9 (ADH_Out[5], ADH_In[5], ~_0_ADH17);  // AND_Gate
  and and_10 (ADH_Out[6], ADH_In[6], ~_0_ADH17);  // AND_Gate
  and and_11 (ADH_Out[7], ADH_In[7], ~_0_ADH17);  // AND_Gate

  assign ADL_Out[7:3] = ADL_In[7:3];
endmodule

module BUS_MUX_HACK (
  input  Y_SB,
  input  X_SB,
  input  S_SB,
  input  AC_DB,
  input  AC_SB,
  input  ADD_SB06,
  input  ADD_SB7,
  input  PCL_DB,
  input  PCH_DB,
  input  PCH_ADH,
  input  DL_ADH,
  input  DL_DB,
  output SB_Dirty,
  output DB_Dirty,
  output ADH_Dirty,
  output SBDB_Clutch
);

  wire or_1_out, or_2_out, or_3_out;

  or or_1 (or_1_out, ADD_SB06, ADD_SB7);
  or or_2 (or_2_out, Y_SB, X_SB, S_SB, AC_SB, or_1_out);
  or or_3 (or_3_out, AC_DB, PCL_DB, PCH_DB, DL_DB);
  or or_4 (ADH_Dirty, PCH_ADH, DL_ADH);
  and and_1 (SBDB_Clutch, or_2_out, or_3_out);
  Multiplexer multiplexer_1 (.in0(or_2_out), .in1(1'b0), .out(SB_Dirty), .sel(SBDB_Clutch));  // open: en
  Multiplexer multiplexer_2 (.in0(or_3_out), .in1(1'b0), .out(DB_Dirty), .sel(SBDB_Clutch));  // open: en
endmodule

module D_Latch (
  input  EN,
  input  D,
  output Q,
  output NOT_Q
);

  D_Flip_Flop #(.trigger("high")) d_ff_1 (.clk(EN), .D(D), .Q(Q), .Qn(NOT_Q));  // open: preset, en, reset
endmodule

module DFF_Level (
  input  EN,
  input  D,
  output Q,
  output NOT_Q
);

  D_Flip_Flop #(.trigger("high")) d_ff_1 (.clk(EN), .D(D), .Q(Q), .Qn(NOT_Q));  // open: preset, en, reset

  // Notes on the sheet:
  //   To simplify importing into Logisim Evo.
endmodule

module DFF_Posedge (
  input  EN,
  input  D,
  output Q,
  output NOT_Q
);

  D_Flip_Flop #(.trigger("falling")) d_ff_1 (.clk(EN), .D(D), .Q(Q), .Qn(NOT_Q));  // open: preset, en, reset

  // Notes on the sheet:
  //   posedge
  //   To simplify importing into Logisim Evo.
endmodule
