// Logisim project 6502_Evo.circ as structural Verilog: 46 circuits, main circuit BogusSystem
module BogusSystem (
  input  RDY,
  input  SO,
  input  L_NMI_153cf1a9,
  input  L_IRQ_ec2f2199,
  input  L_RES_2d8f5153
);

  wire l_6502_c0de69bb_1_phi2, l_6502_c0de69bb_1_r_w_0418701b, not_1_out, PHI0_out;
  wire [7:0] l_6502_c0de69bb_1_out_27, ram_1_dout;
  wire [15:0] l_6502_c0de69bb_1_a0;

  Clock PHI0 (.out(PHI0_out));
  L_6502_c0de69bb l_6502_c0de69bb_1 (
    .PHI2(l_6502_c0de69bb_1_phi2), .R_W_0418701b(l_6502_c0de69bb_1_r_w_0418701b),
    .out_27(l_6502_c0de69bb_1_out_27[0]), .D1(l_6502_c0de69bb_1_out_27[1]), .D2(l_6502_c0de69bb_1_out_27[2]),
    .out_30(l_6502_c0de69bb_1_out_27[3]), .out_31(l_6502_c0de69bb_1_out_27[4]),
    .D5(l_6502_c0de69bb_1_out_27[5]), .out_41(l_6502_c0de69bb_1_out_27[6]),
    .out_42(l_6502_c0de69bb_1_out_27[7]), .A8(l_6502_c0de69bb_1_a0[8]), .A9(l_6502_c0de69bb_1_a0[9]),
    .A10(l_6502_c0de69bb_1_a0[10]), .A11(l_6502_c0de69bb_1_a0[11]), .A12(l_6502_c0de69bb_1_a0[12]),
    .A13(l_6502_c0de69bb_1_a0[13]), .A14(l_6502_c0de69bb_1_a0[14]), .A0(l_6502_c0de69bb_1_a0[0]),
    .A1(l_6502_c0de69bb_1_a0[1]), .A2(l_6502_c0de69bb_1_a0[2]), .A3(l_6502_c0de69bb_1_a0[3]),
    .A4(l_6502_c0de69bb_1_a0[4]), .A5(l_6502_c0de69bb_1_a0[5]), .A6(l_6502_c0de69bb_1_a0[6]),
    .A7(l_6502_c0de69bb_1_a0[7]), .A15(l_6502_c0de69bb_1_a0[15]), .L_RES_2d8f5153(L_RES_2d8f5153), .SO(SO),
    .PHI0(PHI0_out), .D0(ram_1_dout[0]), .in_8(ram_1_dout[1]), .in_9(ram_1_dout[2]), .D3(ram_1_dout[3]),
    .D4(ram_1_dout[4]), .in_12(ram_1_dout[5]), .D6(ram_1_dout[6]), .D7(ram_1_dout[7]),
    .L_NMI_153cf1a9(L_NMI_153cf1a9), .L_IRQ_ec2f2199(L_IRQ_ec2f2199), .RDY(RDY));  // open: SYNC, PHI1
  not not_1 (not_1_out, l_6502_c0de69bb_1_r_w_0418701b);
  RAM #(.addrWidth(16)) ram_1 (
    .addr(l_6502_c0de69bb_1_a0), .we(not_1_out), .oe(l_6502_c0de69bb_1_r_w_0418701b),
    .clk(l_6502_c0de69bb_1_phi2), .din(l_6502_c0de69bb_1_out_27), .dout(ram_1_dout));
endmodule

module L_6502_c0de69bb (
  input  L_NMI_153cf1a9,
  input  L_IRQ_ec2f2199,
  input  RDY,
  input  L_RES_2d8f5153,
  input  SO,
  input  PHI0,
  input  D0,
  input  in_8,
  input  in_9,
  input  D3,
  input  D4,
  input  in_12,
  input  D6,
  input  D7,
  output PHI1,
  output PHI2,
  output R_W_0418701b,
  output SYNC,
  output A0,
  output A1,
  output A2,
  output A3,
  output A4,
  output A5,
  output A6,
  output A7,
  output out_27,
  output D1,
  output D2,
  output out_30,
  output out_31,
  output D5,
  output A8,
  output A9,
  output A10,
  output A11,
  output A12,
  output A13,
  output A14,
  output A15,
  output out_41,
  output out_42
);

  wire alu_1_acr, alu_1_avr, d_ff_1_qn, d_ff_2_qn, d_ff_3_q, decoder_trans_1_l_0_4ba6ff26,
       decoder_trans_1_l_1_3b22cb4c, decoder_trans_1_l_2_4a831fe0, decoder_trans_1_l_3_16a57085,
       decoder_trans_1_l_4_45284221, decoder_trans_1_l_5_79aea93e, decoder_trans_1_l_6_420976ce,
       decoder_trans_1_l_7_6f2638d9, decoder_trans_1_l_8_129a8ae9, decoder_trans_1_l_9_953a8f61,
       decoder_trans_1_l_10_6da465ad, decoder_trans_1_l_11_4ca67c7e, decoder_trans_1_l_12_142439c6,
       decoder_trans_1_l_13_20e8ba47, decoder_trans_1_l_14_5208a13d, decoder_trans_1_l_15_991215f6,
       decoder_trans_1_l_16_663400da, decoder_trans_1_l_17_d2862fba, decoder_trans_1_l_18_04a5e6fc,
       decoder_trans_1_l_19_7b271e4d, decoder_trans_1_l_20_8c61ee26, decoder_trans_1_l_21_feeca76b,
       decoder_trans_1_l_22_7a606cb8, decoder_trans_1_l_23_91cdc8b5, decoder_trans_1_l_24_62a90c42,
       decoder_trans_1_l_25_ec7c8b92, decoder_trans_1_l_26_4792594e, decoder_trans_1_l_27_bffb8973,
       decoder_trans_1_l_28_d2630233, decoder_trans_1_l_29_28b5b79d, decoder_trans_1_l_30_13bc78e9,
       decoder_trans_1_l_31_d65b4f16, decoder_trans_1_l_32_a76bc5d3, decoder_trans_1_l_33_4c80d111,
       decoder_trans_1_l_34_ec404986, decoder_trans_1_l_35_a3ad9e97, decoder_trans_1_l_36_f906ff59,
       decoder_trans_1_l_37_970560ea, decoder_trans_1_l_38_44e13d1d, decoder_trans_1_l_39_ab49266d,
       decoder_trans_1_l_40_b0ce7c4d, decoder_trans_1_l_41_5ba99609, decoder_trans_1_l_42_05de627d,
       decoder_trans_1_l_43_e53210b4, decoder_trans_1_l_44_7557d7f6, decoder_trans_1_l_45_d477530d,
       decoder_trans_1_l_46_8026585c, decoder_trans_1_l_47_50b9384c, decoder_trans_1_l_48_961f2eda,
       decoder_trans_1_l_49_b961b159, decoder_trans_1_l_50_7cd0b929, decoder_trans_1_l_51_73afc739,
       decoder_trans_1_l_52_6bbb5c5f, decoder_trans_1_l_53_db17dfc3, decoder_trans_1_l_54_df2d9682,
       decoder_trans_1_l_55_9656bee7, decoder_trans_1_l_56_ff4a974b, decoder_trans_1_l_57_bd139f3f,
       decoder_trans_1_l_58_b698ce08, decoder_trans_1_l_59_15390865, decoder_trans_1_l_60_ba37dadc,
       decoder_trans_1_l_61_aa3c3e0c, decoder_trans_1_l_62_1cf1b605, decoder_trans_1_l_63_0219edaa,
       decoder_trans_1_l_64_c9babf32, decoder_trans_1_l_65_a97300ad, decoder_trans_1_l_66_53023e8d,
       decoder_trans_1_l_67_07e7e8b6, decoder_trans_1_l_68_a93b1446, decoder_trans_1_l_69_c6a8c7bd,
       decoder_trans_1_l_70_14a93969, decoder_trans_1_l_71_037940dd, decoder_trans_1_l_72_65280ac2,
       decoder_trans_1_l_73_116545e2, decoder_trans_1_l_74_8a887fe0, decoder_trans_1_l_75_fbc631d3,
       decoder_trans_1_l_76_0c9e8790, decoder_trans_1_l_77_8a8d3736, decoder_trans_1_l_78_142fff2c,
       decoder_trans_1_l_79_88caeb61, decoder_trans_1_l_80_442d40a3, decoder_trans_1_l_81_7ac19b4f,
       decoder_trans_1_l_82_53fd2612, decoder_trans_1_l_83_8900340a, decoder_trans_1_l_84_4e42f7b7,
       decoder_trans_1_l_85_90e036dc, decoder_trans_1_l_86_fae89fad, decoder_trans_1_l_87_be04a52b,
       decoder_trans_1_l_88_ae4b2cef, decoder_trans_1_l_89_f62eed49, decoder_trans_1_l_90_d21e06c7,
       decoder_trans_1_l_91_1b0c0c3e, decoder_trans_1_l_92_0642b8ec, decoder_trans_1_l_93_66c1bc08,
       decoder_trans_1_l_94_c36cbd45, decoder_trans_1_l_95_8b08e919, decoder_trans_1_l_96_4be017a7,
       decoder_trans_1_l_97_91c265e2, decoder_trans_1_l_98_1dfb9b6f, decoder_trans_1_l_99_0cc83ca0,
       decoder_trans_1_l_100_35836628, decoder_trans_1_l_101_9d393967, decoder_trans_1_l_102_881ca15e,
       decoder_trans_1_l_103_46ba03e4, decoder_trans_1_l_104_2077d36b, decoder_trans_1_l_105_a29cdf8d,
       decoder_trans_1_l_106_36001eab, decoder_trans_1_l_107_68d37105, decoder_trans_1_l_108_a15fa495,
       decoder_trans_1_l_109_8b0ee0a1, decoder_trans_1_l_110_e7c60ed0, decoder_trans_1_l_111_1042ad89,
       decoder_trans_1_l_112_063f5ab4, decoder_trans_1_l_113_69d8438b, decoder_trans_1_l_114_a7bf33c8,
       decoder_trans_1_l_115_0ffd4dd7, decoder_trans_1_l_116_f87463c5, decoder_trans_1_l_117_54ea7dab,
       decoder_trans_1_l_118_25ed7443, decoder_trans_1_l_119_bc2ca239, decoder_trans_1_l_120_bf62daef,
       decoder_trans_1_l_121_348bd5c4, decoder_trans_1_l_122_2b9e98b2, decoder_trans_1_l_123_ea048c49,
       decoder_trans_1_l_124_3cfed9ae, decoder_trans_1_l_125_0b8e34b8, decoder_trans_1_l_126_b55b24f6,
       decoder_trans_1_l_127_f6767dc7, decoder_trans_1_l_128_aad3a25e, decoder_trans_1_l_129_8838ebbd,
       ir_1_ir0, ir_1_ir1, ir_1_ir2, ir_1_ir3, ir_1_ir4, ir_1_ir5, ir_1_ir6, ir_1_ir7, irqp_latch_not_q,
       not_1_out, not_2_out, not_3_out, prdy_latch1_not_q, prdy_latch2_not_q, predecode_1_l_implied_7f832bff,
       predecode_1_l_pd0_72855f64, predecode_1_l_pd1_c99f14c8, predecode_1_l_pd2_8bc41618,
       predecode_1_l_pd3_ba6a24ea, predecode_1_l_pd4_9583460c, predecode_1_l_pd5_8dc63d2b,
       predecode_1_l_pd6_87750ded, predecode_1_l_pd7_40cf097f, predecode_1_l_twocycle_43089fae,
       random_logic_1_acr_c_fc5559e8, random_logic_1_db_c_acfbba71, random_logic_1_db_n_4f1ad326,
       random_logic_1_db_p_0fe10735, random_logic_1_db_v_9eaeb3a2, random_logic_1_dbz_z_805d2a94,
       random_logic_1_ends, random_logic_1_endx, random_logic_1_fetch, random_logic_1_ir5_c_bb157132,
       random_logic_1_ir5_d_a37efeb0, random_logic_1_ir5_i_a8b17eb4, random_logic_1_l_0_ir_fde7bd13,
       random_logic_1_l_0_v_6d5b0af2, random_logic_1_l_c_out_e01a0d59, random_logic_1_l_d_out_eaa1b777,
       random_logic_1_l_i_out_a88ea15a, random_logic_1_l_n_out_f0a30453, random_logic_1_l_t0_be2341f9,
       random_logic_1_l_t1x_cd47d06e, random_logic_1_l_t2_2b20ddce, random_logic_1_l_t3_2730c10f,
       random_logic_1_l_t4_1ff9fe8e, random_logic_1_l_t5_e9d210fb, random_logic_1_l_v_out_cf6c2405,
       random_logic_1_l_z_out_273329d7, random_logic_1_p_db_0ea80532, random_logic_1_t1,
       random_logic_1_tres1, random_logic_1_tres2, random_logic_1_tresx, random_logic_1_wr, resp_latch_not_q;
  wire [1:0] random_logic_1_adh_abh_4fac1902;
  wire [2:0] random_logic_1_dl_adl_73e48c13, random_logic_1_l_acin_e8912140;
  wire [4:0] random_logic_1_l_0_adl0_372ea1ce, random_logic_1_sb_adh_3fc727a4;
  wire [7:0] alu_1_ac_debug, alu_1_add_debug, alu_1_adh0, alu_1_ai_debug, alu_1_bi_debug,
       const_gen_1_adh_out, const_gen_1_adl_out, dl_1_dl_debug, dl_1_dor_debug, precharge_1_adh_out,
       precharge_1_adl_out, precharge_1_db_out, precharge_1_sb_out, random_logic_1_db0,
       random_logic_1_y_sb_981fc62c, regs_1_adl0, regs_1_out_18, regs_1_s_debug, regs_1_x_debug,
       regs_1_y_debug;
  wire [8:0] random_logic_1_adh_pch_413c8ef5;
  wire [12:0] random_logic_1_ndb_add_5826378a;
  wire [15:0] pc_1_pc_debug, pc_1_pcs_debug;

  PRECHARGE precharge_1 (
    .SB_Out(precharge_1_sb_out), .DB_Out(precharge_1_db_out), .ADL_Out(precharge_1_adl_out),
    .ADH_Out(precharge_1_adh_out), .SB_In(regs_1_out_18), .DB_In(random_logic_1_db0), .ADL_In(regs_1_adl0),
    .ADH_In(alu_1_adh0));
  buf buffer_1 (SYNC, random_logic_1_t1);
  CONST_GEN const_gen_1 (
    .ADH_Out(const_gen_1_adh_out), .ADL_Out(const_gen_1_adl_out),
    .L_0_ADL1_1828b789(random_logic_1_l_0_adl0_372ea1ce[1]),
    .L_0_ADL2_a1d2ebaa(random_logic_1_l_0_adl0_372ea1ce[2]),
    .L_0_ADH0_8d3f04fb(random_logic_1_l_0_adl0_372ea1ce[3]),
    .L_0_ADH17_42b6e0bd(random_logic_1_l_0_adl0_372ea1ce[4]),
    .L_0_ADL0_372ea1ce(random_logic_1_l_0_adl0_372ea1ce[0]), .ADH_In(precharge_1_adh_out),
    .ADL_In(precharge_1_adl_out));
  D_Flip_Flop #(.trigger("high")) d_ff_1 (.D(L_NMI_153cf1a9), .clk(PHI2), .Qn(d_ff_1_qn));  // open: Q, preset, reset
  DECODER_TRANS decoder_trans_1 (
    .L_10_6da465ad(decoder_trans_1_l_10_6da465ad), .L_11_4ca67c7e(decoder_trans_1_l_11_4ca67c7e),
    .L_12_142439c6(decoder_trans_1_l_12_142439c6), .L_13_20e8ba47(decoder_trans_1_l_13_20e8ba47),
    .L_14_5208a13d(decoder_trans_1_l_14_5208a13d), .L_15_991215f6(decoder_trans_1_l_15_991215f6),
    .L_16_663400da(decoder_trans_1_l_16_663400da), .L_17_d2862fba(decoder_trans_1_l_17_d2862fba),
    .L_18_04a5e6fc(decoder_trans_1_l_18_04a5e6fc), .L_19_7b271e4d(decoder_trans_1_l_19_7b271e4d),
    .L_20_8c61ee26(decoder_trans_1_l_20_8c61ee26), .L_21_feeca76b(decoder_trans_1_l_21_feeca76b),
    .L_22_7a606cb8(decoder_trans_1_l_22_7a606cb8), .L_23_91cdc8b5(decoder_trans_1_l_23_91cdc8b5),
    .L_24_62a90c42(decoder_trans_1_l_24_62a90c42), .L_25_ec7c8b92(decoder_trans_1_l_25_ec7c8b92),
    .L_26_4792594e(decoder_trans_1_l_26_4792594e), .L_27_bffb8973(decoder_trans_1_l_27_bffb8973),
    .L_28_d2630233(decoder_trans_1_l_28_d2630233), .L_29_28b5b79d(decoder_trans_1_l_29_28b5b79d),
    .L_30_13bc78e9(decoder_trans_1_l_30_13bc78e9), .L_31_d65b4f16(decoder_trans_1_l_31_d65b4f16),
    .L_32_a76bc5d3(decoder_trans_1_l_32_a76bc5d3), .L_33_4c80d111(decoder_trans_1_l_33_4c80d111),
    .L_34_ec404986(decoder_trans_1_l_34_ec404986), .L_35_a3ad9e97(decoder_trans_1_l_35_a3ad9e97),
    .L_36_f906ff59(decoder_trans_1_l_36_f906ff59), .L_37_970560ea(decoder_trans_1_l_37_970560ea),
    .L_38_44e13d1d(decoder_trans_1_l_38_44e13d1d), .L_39_ab49266d(decoder_trans_1_l_39_ab49266d),
    .L_40_b0ce7c4d(decoder_trans_1_l_40_b0ce7c4d), .L_41_5ba99609(decoder_trans_1_l_41_5ba99609),
    .L_42_05de627d(decoder_trans_1_l_42_05de627d), .L_43_e53210b4(decoder_trans_1_l_43_e53210b4),
    .L_44_7557d7f6(decoder_trans_1_l_44_7557d7f6), .L_0_4ba6ff26(decoder_trans_1_l_0_4ba6ff26),
    .L_45_d477530d(decoder_trans_1_l_45_d477530d), .L_46_8026585c(decoder_trans_1_l_46_8026585c),
    .L_47_50b9384c(decoder_trans_1_l_47_50b9384c), .L_48_961f2eda(decoder_trans_1_l_48_961f2eda),
    .L_49_b961b159(decoder_trans_1_l_49_b961b159), .L_50_7cd0b929(decoder_trans_1_l_50_7cd0b929),
    .L_51_73afc739(decoder_trans_1_l_51_73afc739), .L_52_6bbb5c5f(decoder_trans_1_l_52_6bbb5c5f),
    .L_53_db17dfc3(decoder_trans_1_l_53_db17dfc3), .L_1_3b22cb4c(decoder_trans_1_l_1_3b22cb4c),
    .L_54_df2d9682(decoder_trans_1_l_54_df2d9682), .L_55_9656bee7(decoder_trans_1_l_55_9656bee7),
    .L_56_ff4a974b(decoder_trans_1_l_56_ff4a974b), .L_57_bd139f3f(decoder_trans_1_l_57_bd139f3f),
    .L_58_b698ce08(decoder_trans_1_l_58_b698ce08), .L_59_15390865(decoder_trans_1_l_59_15390865),
    .L_60_ba37dadc(decoder_trans_1_l_60_ba37dadc), .L_61_aa3c3e0c(decoder_trans_1_l_61_aa3c3e0c),
    .L_62_1cf1b605(decoder_trans_1_l_62_1cf1b605), .L_2_4a831fe0(decoder_trans_1_l_2_4a831fe0),
    .L_63_0219edaa(decoder_trans_1_l_63_0219edaa), .L_64_c9babf32(decoder_trans_1_l_64_c9babf32),
    .L_65_a97300ad(decoder_trans_1_l_65_a97300ad), .L_66_53023e8d(decoder_trans_1_l_66_53023e8d),
    .L_67_07e7e8b6(decoder_trans_1_l_67_07e7e8b6), .L_68_a93b1446(decoder_trans_1_l_68_a93b1446),
    .L_69_c6a8c7bd(decoder_trans_1_l_69_c6a8c7bd), .L_70_14a93969(decoder_trans_1_l_70_14a93969),
    .L_71_037940dd(decoder_trans_1_l_71_037940dd), .L_72_65280ac2(decoder_trans_1_l_72_65280ac2),
    .L_3_16a57085(decoder_trans_1_l_3_16a57085), .L_73_116545e2(decoder_trans_1_l_73_116545e2),
    .L_74_8a887fe0(decoder_trans_1_l_74_8a887fe0), .L_75_fbc631d3(decoder_trans_1_l_75_fbc631d3),
    .L_76_0c9e8790(decoder_trans_1_l_76_0c9e8790), .L_77_8a8d3736(decoder_trans_1_l_77_8a8d3736),
    .L_78_142fff2c(decoder_trans_1_l_78_142fff2c), .L_79_88caeb61(decoder_trans_1_l_79_88caeb61),
    .L_80_442d40a3(decoder_trans_1_l_80_442d40a3), .L_81_7ac19b4f(decoder_trans_1_l_81_7ac19b4f),
    .L_4_45284221(decoder_trans_1_l_4_45284221), .L_82_53fd2612(decoder_trans_1_l_82_53fd2612),
    .L_83_8900340a(decoder_trans_1_l_83_8900340a), .L_84_4e42f7b7(decoder_trans_1_l_84_4e42f7b7),
    .L_85_90e036dc(decoder_trans_1_l_85_90e036dc), .L_86_fae89fad(decoder_trans_1_l_86_fae89fad),
    .L_87_be04a52b(decoder_trans_1_l_87_be04a52b), .L_88_ae4b2cef(decoder_trans_1_l_88_ae4b2cef),
    .L_89_f62eed49(decoder_trans_1_l_89_f62eed49), .L_90_d21e06c7(decoder_trans_1_l_90_d21e06c7),
    .L_5_79aea93e(decoder_trans_1_l_5_79aea93e), .L_91_1b0c0c3e(decoder_trans_1_l_91_1b0c0c3e),
    .L_92_0642b8ec(decoder_trans_1_l_92_0642b8ec), .L_93_66c1bc08(decoder_trans_1_l_93_66c1bc08),
    .L_94_c36cbd45(decoder_trans_1_l_94_c36cbd45), .L_95_8b08e919(decoder_trans_1_l_95_8b08e919),
    .L_96_4be017a7(decoder_trans_1_l_96_4be017a7), .L_97_91c265e2(decoder_trans_1_l_97_91c265e2),
    .L_98_1dfb9b6f(decoder_trans_1_l_98_1dfb9b6f), .L_99_0cc83ca0(decoder_trans_1_l_99_0cc83ca0),
    .L_100_35836628(decoder_trans_1_l_100_35836628), .L_101_9d393967(decoder_trans_1_l_101_9d393967),
    .L_102_881ca15e(decoder_trans_1_l_102_881ca15e), .L_103_46ba03e4(decoder_trans_1_l_103_46ba03e4),
    .L_104_2077d36b(decoder_trans_1_l_104_2077d36b), .L_105_a29cdf8d(decoder_trans_1_l_105_a29cdf8d),
    .L_106_36001eab(decoder_trans_1_l_106_36001eab), .L_107_68d37105(decoder_trans_1_l_107_68d37105),
    .L_108_a15fa495(decoder_trans_1_l_108_a15fa495), .L_109_8b0ee0a1(decoder_trans_1_l_109_8b0ee0a1),
    .L_6_420976ce(decoder_trans_1_l_6_420976ce), .L_110_e7c60ed0(decoder_trans_1_l_110_e7c60ed0),
    .L_111_1042ad89(decoder_trans_1_l_111_1042ad89), .L_112_063f5ab4(decoder_trans_1_l_112_063f5ab4),
    .L_113_69d8438b(decoder_trans_1_l_113_69d8438b), .L_114_a7bf33c8(decoder_trans_1_l_114_a7bf33c8),
    .L_115_0ffd4dd7(decoder_trans_1_l_115_0ffd4dd7), .L_116_f87463c5(decoder_trans_1_l_116_f87463c5),
    .L_117_54ea7dab(decoder_trans_1_l_117_54ea7dab), .L_118_25ed7443(decoder_trans_1_l_118_25ed7443),
    .L_119_bc2ca239(decoder_trans_1_l_119_bc2ca239), .L_7_6f2638d9(decoder_trans_1_l_7_6f2638d9),
    .L_120_bf62daef(decoder_trans_1_l_120_bf62daef), .L_121_348bd5c4(decoder_trans_1_l_121_348bd5c4),
    .L_122_2b9e98b2(decoder_trans_1_l_122_2b9e98b2), .L_123_ea048c49(decoder_trans_1_l_123_ea048c49),
    .L_124_3cfed9ae(decoder_trans_1_l_124_3cfed9ae), .L_125_0b8e34b8(decoder_trans_1_l_125_0b8e34b8),
    .L_126_b55b24f6(decoder_trans_1_l_126_b55b24f6), .L_127_f6767dc7(decoder_trans_1_l_127_f6767dc7),
    .L_128_aad3a25e(decoder_trans_1_l_128_aad3a25e), .L_129_8838ebbd(decoder_trans_1_l_129_8838ebbd),
    .L_8_129a8ae9(decoder_trans_1_l_8_129a8ae9), .L_9_953a8f61(decoder_trans_1_l_9_953a8f61), .IR6(ir_1_ir6),
    .IR5(ir_1_ir5), .L_T0_be2341f9(random_logic_1_l_t0_be2341f9),
    .L_T1X_cd47d06e(random_logic_1_l_t1x_cd47d06e), .L_T5_e9d210fb(random_logic_1_l_t5_e9d210fb),
    .L_T4_1ff9fe8e(random_logic_1_l_t4_1ff9fe8e), .L_T3_2730c10f(random_logic_1_l_t3_2730c10f),
    .L_T2_2b20ddce(random_logic_1_l_t2_2b20ddce), .IR0(ir_1_ir0), .IR1(ir_1_ir1), .IR7(ir_1_ir7),
    .IR4(ir_1_ir4), .IR3(ir_1_ir3), .IR2(ir_1_ir2));
  RANDOM_LOGIC random_logic_1 (
    .L_N_OUT_f0a30453(random_logic_1_l_n_out_f0a30453), .L_Z_OUT_273329d7(random_logic_1_l_z_out_273329d7),
    .NDB_ADD_5826378a(random_logic_1_ndb_add_5826378a[0]),
    .DB_ADD_49072aec(random_logic_1_ndb_add_5826378a[1]),
    .L_0_ADD_7d0d5e3b(random_logic_1_ndb_add_5826378a[2]),
    .SB_ADD_21cc08e7(random_logic_1_ndb_add_5826378a[3]),
    .ADL_ADD_b3e2e6b8(random_logic_1_ndb_add_5826378a[4]), .ANDS(random_logic_1_ndb_add_5826378a[8]),
    .EORS(random_logic_1_ndb_add_5826378a[9]), .ORS(random_logic_1_ndb_add_5826378a[10]),
    .L_ACIN_e8912140(random_logic_1_l_acin_e8912140[0]), .SUMS(random_logic_1_ndb_add_5826378a[12]),
    .L_DAA_9902be4a(random_logic_1_l_acin_e8912140[1]),
    .ADD_SB7_3b72c6f5(random_logic_1_ndb_add_5826378a[6]),
    .ADD_SB06_79b3146b(random_logic_1_ndb_add_5826378a[5]),
    .ADD_ADL_d25cdcd8(random_logic_1_ndb_add_5826378a[7]),
    .L_DSA_8e87f2a8(random_logic_1_l_acin_e8912140[2]), .SRS(random_logic_1_ndb_add_5826378a[11]),
    .DL_ADL_73e48c13(random_logic_1_dl_adl_73e48c13[0]), .DL_DB_4a6f16a8(random_logic_1_dl_adl_73e48c13[1]),
    .DL_ADH_067137e0(random_logic_1_dl_adl_73e48c13[2]),
    .ADH_ABH_4fac1902(random_logic_1_adh_abh_4fac1902[0]),
    .L_0_ADL0_372ea1ce(random_logic_1_l_0_adl0_372ea1ce[0]),
    .ADL_ABL_ccbf1bfb(random_logic_1_adh_abh_4fac1902[1]),
    .SB_AC_692b76aa(random_logic_1_sb_adh_3fc727a4[4]), .AC_SB_4f3a8e20(random_logic_1_sb_adh_3fc727a4[3]),
    .L_0_ADH0_8d3f04fb(random_logic_1_l_0_adl0_372ea1ce[3]),
    .L_0_ADH17_42b6e0bd(random_logic_1_l_0_adl0_372ea1ce[4]),
    .AC_DB_7461a43f(random_logic_1_sb_adh_3fc727a4[2]), .SB_DB_92ea0e91(random_logic_1_sb_adh_3fc727a4[1]),
    .SB_ADH_3fc727a4(random_logic_1_sb_adh_3fc727a4[0]),
    .L_0_ADL1_1828b789(random_logic_1_l_0_adl0_372ea1ce[1]),
    .ADL_PCL_0d330abd(random_logic_1_adh_pch_413c8ef5[4]),
    .PCL_PCL_effd7227(random_logic_1_adh_pch_413c8ef5[5]),
    .PCH_ADH_329c7fb7(random_logic_1_adh_pch_413c8ef5[2]),
    .PCL_ADL_75837bef(random_logic_1_adh_pch_413c8ef5[6]),
    .PCH_DB_4d5eb992(random_logic_1_adh_pch_413c8ef5[3]),
    .PCL_DB_8c5417e4(random_logic_1_adh_pch_413c8ef5[7]),
    .ADH_PCH_413c8ef5(random_logic_1_adh_pch_413c8ef5[0]),
    .PCH_PCH_e0d1ea0f(random_logic_1_adh_pch_413c8ef5[1]),
    .L_0_ADL2_a1d2ebaa(random_logic_1_l_0_adl0_372ea1ce[2]), .TRESX(random_logic_1_tresx),
    .L_0_IR_fde7bd13(random_logic_1_l_0_ir_fde7bd13), .ENDS(random_logic_1_ends), .ENDX(random_logic_1_endx),
    .TRES1(random_logic_1_tres1), .T1(random_logic_1_t1), .L_T1X_cd47d06e(random_logic_1_l_t1x_cd47d06e),
    .TRES2(random_logic_1_tres2), .L_1_PC_f7ea2184(random_logic_1_adh_pch_413c8ef5[8]),
    .Y_SB_981fc62c(random_logic_1_y_sb_981fc62c[0]), .P_DB_0ea80532(random_logic_1_p_db_0ea80532),
    .IR5_I_a8b17eb4(random_logic_1_ir5_i_a8b17eb4), .IR5_C_bb157132(random_logic_1_ir5_c_bb157132),
    .IR5_D_a37efeb0(random_logic_1_ir5_d_a37efeb0), .L_0_V_6d5b0af2(random_logic_1_l_0_v_6d5b0af2),
    .out_232(random_logic_1_db0[7]), .ACR_C_fc5559e8(random_logic_1_acr_c_fc5559e8),
    .DB6(random_logic_1_db0[6]), .DBZ_Z_805d2a94(random_logic_1_dbz_z_805d2a94),
    .out_234(random_logic_1_db0[5]), .DB_N_4f1ad326(random_logic_1_db_n_4f1ad326),
    .out_235(random_logic_1_db0[4]), .DB_P_0fe10735(random_logic_1_db_p_0fe10735),
    .DB3(random_logic_1_db0[3]), .DB_C_acfbba71(random_logic_1_db_c_acfbba71), .DB2(random_logic_1_db0[2]),
    .DB_V_9eaeb3a2(random_logic_1_db_v_9eaeb3a2), .DB1(random_logic_1_db0[1]), .DB0(random_logic_1_db0[0]),
    .X_SB_50e8fb84(random_logic_1_y_sb_981fc62c[2]), .L_T3_2730c10f(random_logic_1_l_t3_2730c10f),
    .L_T4_1ff9fe8e(random_logic_1_l_t4_1ff9fe8e), .L_T5_e9d210fb(random_logic_1_l_t5_e9d210fb),
    .WR(random_logic_1_wr), .FETCH(random_logic_1_fetch), .L_T0_be2341f9(random_logic_1_l_t0_be2341f9),
    .L_T2_2b20ddce(random_logic_1_l_t2_2b20ddce), .SB_Y_f952d371(random_logic_1_y_sb_981fc62c[1]),
    .SB_X_a4a389b1(random_logic_1_y_sb_981fc62c[3]), .S_SB_c8f0deaa(random_logic_1_y_sb_981fc62c[7]),
    .S_ADL_299349f9(random_logic_1_y_sb_981fc62c[4]), .SB_S_e7e7b943(random_logic_1_y_sb_981fc62c[6]),
    .S_S_0e77937e(random_logic_1_y_sb_981fc62c[5]), .L_V_OUT_cf6c2405(random_logic_1_l_v_out_cf6c2405),
    .L_I_OUT_a88ea15a(random_logic_1_l_i_out_a88ea15a), .L_D_OUT_eaa1b777(random_logic_1_l_d_out_eaa1b777),
    .L_C_OUT_e01a0d59(random_logic_1_l_c_out_e01a0d59), .X28(decoder_trans_1_l_28_d2630233),
    .X29(decoder_trans_1_l_29_28b5b79d), .X30(decoder_trans_1_l_30_13bc78e9),
    .X31(decoder_trans_1_l_31_d65b4f16), .X32(decoder_trans_1_l_32_a76bc5d3),
    .X0(decoder_trans_1_l_0_4ba6ff26), .X33(decoder_trans_1_l_33_4c80d111),
    .X34(decoder_trans_1_l_34_ec404986), .X35(decoder_trans_1_l_35_a3ad9e97),
    .X36(decoder_trans_1_l_36_f906ff59), .X37(decoder_trans_1_l_37_970560ea),
    .X38(decoder_trans_1_l_38_44e13d1d), .X39(decoder_trans_1_l_39_ab49266d),
    .X40(decoder_trans_1_l_40_b0ce7c4d), .X41(decoder_trans_1_l_41_5ba99609),
    .X1(decoder_trans_1_l_1_3b22cb4c), .X42(decoder_trans_1_l_42_05de627d),
    .X43(decoder_trans_1_l_43_e53210b4), .X44(decoder_trans_1_l_44_7557d7f6),
    .X45(decoder_trans_1_l_45_d477530d), .X46(decoder_trans_1_l_46_8026585c),
    .X47(decoder_trans_1_l_47_50b9384c), .X48(decoder_trans_1_l_48_961f2eda),
    .X49(decoder_trans_1_l_49_b961b159), .X50(decoder_trans_1_l_50_7cd0b929),
    .X2(decoder_trans_1_l_2_4a831fe0), .X51(decoder_trans_1_l_51_73afc739),
    .X52(decoder_trans_1_l_52_6bbb5c5f), .X53(decoder_trans_1_l_53_db17dfc3),
    .X54(decoder_trans_1_l_54_df2d9682), .X55(decoder_trans_1_l_55_9656bee7),
    .X56(decoder_trans_1_l_56_ff4a974b), .X57(decoder_trans_1_l_57_bd139f3f),
    .X58(decoder_trans_1_l_58_b698ce08), .X59(decoder_trans_1_l_59_15390865),
    .X3(decoder_trans_1_l_3_16a57085), .X60(decoder_trans_1_l_60_ba37dadc),
    .X61(decoder_trans_1_l_61_aa3c3e0c), .X62(decoder_trans_1_l_62_1cf1b605),
    .X63(decoder_trans_1_l_63_0219edaa), .X64(decoder_trans_1_l_64_c9babf32),
    .X65(decoder_trans_1_l_65_a97300ad), .X66(decoder_trans_1_l_66_53023e8d),
    .X67(decoder_trans_1_l_67_07e7e8b6), .X68(decoder_trans_1_l_68_a93b1446),
    .X69(decoder_trans_1_l_69_c6a8c7bd), .X4(decoder_trans_1_l_4_45284221),
    .X70(decoder_trans_1_l_70_14a93969), .X71(decoder_trans_1_l_71_037940dd),
    .X72(decoder_trans_1_l_72_65280ac2), .X73(decoder_trans_1_l_73_116545e2),
    .X74(decoder_trans_1_l_74_8a887fe0), .X75(decoder_trans_1_l_75_fbc631d3),
    .X76(decoder_trans_1_l_76_0c9e8790), .X77(decoder_trans_1_l_77_8a8d3736),
    .X78(decoder_trans_1_l_78_142fff2c), .X5(decoder_trans_1_l_5_79aea93e),
    .X79(decoder_trans_1_l_79_88caeb61), .X80(decoder_trans_1_l_80_442d40a3),
    .X81(decoder_trans_1_l_81_7ac19b4f), .X82(decoder_trans_1_l_82_53fd2612),
    .X83(decoder_trans_1_l_83_8900340a), .X84(decoder_trans_1_l_84_4e42f7b7),
    .X85(decoder_trans_1_l_85_90e036dc), .X86(decoder_trans_1_l_86_fae89fad),
    .X87(decoder_trans_1_l_87_be04a52b), .X6(decoder_trans_1_l_6_420976ce),
    .X88(decoder_trans_1_l_88_ae4b2cef), .X89(decoder_trans_1_l_89_f62eed49),
    .X90(decoder_trans_1_l_90_d21e06c7), .X91(decoder_trans_1_l_91_1b0c0c3e),
    .X92(decoder_trans_1_l_92_0642b8ec), .X93(decoder_trans_1_l_93_66c1bc08),
    .X94(decoder_trans_1_l_94_c36cbd45), .X95(decoder_trans_1_l_95_8b08e919),
    .X96(decoder_trans_1_l_96_4be017a7), .X7(decoder_trans_1_l_7_6f2638d9),
    .X97(decoder_trans_1_l_97_91c265e2), .X98(decoder_trans_1_l_98_1dfb9b6f),
    .X99(decoder_trans_1_l_99_0cc83ca0), .X100(decoder_trans_1_l_100_35836628),
    .X101(decoder_trans_1_l_101_9d393967), .X102(decoder_trans_1_l_102_881ca15e),
    .X103(decoder_trans_1_l_103_46ba03e4), .X104(decoder_trans_1_l_104_2077d36b),
    .X105(decoder_trans_1_l_105_a29cdf8d), .X8(decoder_trans_1_l_8_129a8ae9),
    .X106(decoder_trans_1_l_106_36001eab), .X107(decoder_trans_1_l_107_68d37105),
    .X108(decoder_trans_1_l_108_a15fa495), .X109(decoder_trans_1_l_109_8b0ee0a1),
    .X110(decoder_trans_1_l_110_e7c60ed0), .X111(decoder_trans_1_l_111_1042ad89),
    .X112(decoder_trans_1_l_112_063f5ab4), .X113(decoder_trans_1_l_113_69d8438b),
    .X114(decoder_trans_1_l_114_a7bf33c8), .X9(decoder_trans_1_l_9_953a8f61),
    .X115(decoder_trans_1_l_115_0ffd4dd7), .X116(decoder_trans_1_l_116_f87463c5),
    .X117(decoder_trans_1_l_117_54ea7dab), .X118(decoder_trans_1_l_118_25ed7443),
    .X119(decoder_trans_1_l_119_bc2ca239), .X120(decoder_trans_1_l_120_bf62daef),
    .X121(decoder_trans_1_l_121_348bd5c4), .X122(decoder_trans_1_l_122_2b9e98b2),
    .X123(decoder_trans_1_l_123_ea048c49), .X124(decoder_trans_1_l_124_3cfed9ae),
    .X125(decoder_trans_1_l_125_0b8e34b8), .X126(decoder_trans_1_l_126_b55b24f6),
    .X127(decoder_trans_1_l_127_f6767dc7), .X128(decoder_trans_1_l_128_aad3a25e),
    .X129(decoder_trans_1_l_129_8838ebbd), .X10(decoder_trans_1_l_10_6da465ad), .DB7(precharge_1_db_out[7]),
    .in_145(precharge_1_db_out[6]), .DB5(precharge_1_db_out[5]), .DB4(precharge_1_db_out[4]),
    .in_148(precharge_1_db_out[3]), .in_149(precharge_1_db_out[2]), .PHI2(PHI2), .L_IR5_7bf6fd52(not_3_out),
    .PHI1(PHI1), .L_TWOCYCLE_43089fae(predecode_1_l_twocycle_43089fae),
    .L_IMPLIED_7f832bff(predecode_1_l_implied_7f832bff), .RDY(RDY), .L_PRDY_7910aae2(prdy_latch2_not_q),
    .in_150(precharge_1_db_out[1]), .in_151(precharge_1_db_out[0]), .X11(decoder_trans_1_l_11_4ca67c7e),
    .X12(decoder_trans_1_l_12_142439c6), .X13(decoder_trans_1_l_13_20e8ba47),
    .X14(decoder_trans_1_l_14_5208a13d), .X15(decoder_trans_1_l_15_991215f6),
    .X16(decoder_trans_1_l_16_663400da), .X17(decoder_trans_1_l_17_d2862fba),
    .X18(decoder_trans_1_l_18_04a5e6fc), .L_NMIP_e9ae5a44(not_1_out), .RESP(resp_latch_not_q),
    .L_IRQP_906cd47b(irqp_latch_not_q), .AVR(alu_1_avr), .ACR(alu_1_acr), .SO(SO),
    .X19(decoder_trans_1_l_19_7b271e4d), .X20(decoder_trans_1_l_20_8c61ee26),
    .X21(decoder_trans_1_l_21_feeca76b), .X22(decoder_trans_1_l_22_7a606cb8),
    .X23(decoder_trans_1_l_23_91cdc8b5), .X24(decoder_trans_1_l_24_62a90c42),
    .X25(decoder_trans_1_l_25_ec7c8b92), .X26(decoder_trans_1_l_26_4792594e),
    .X27(decoder_trans_1_l_27_bffb8973));
  not not_1 (not_1_out, d_ff_1_qn);
  ABL abl_1 (
    .A0(A0), .A1(A1), .A2(A2), .A3(A3), .A4(A4), .A5(A5), .A6(A6), .A7(A7),
    .ADL_ABL_ccbf1bfb(random_logic_1_adh_abh_4fac1902[1]), .ADL0(const_gen_1_adl_out[0]),
    .ADL1(const_gen_1_adl_out[1]), .ADL2(const_gen_1_adl_out[2]), .ADL3(const_gen_1_adl_out[3]), .PHI1(PHI1),
    .ADL4(const_gen_1_adl_out[4]), .ADL5(const_gen_1_adl_out[5]), .ADL6(const_gen_1_adl_out[6]),
    .ADL7(const_gen_1_adl_out[7]), .PHI2(PHI2));
  ABH abh_1 (
    .A8(A8), .A9(A9), .A10(A10), .A11(A11), .A12(A12), .A13(A13), .A14(A14), .A15(A15),
    .ADH_ABH_4fac1902(random_logic_1_adh_abh_4fac1902[0]), .ADH0(const_gen_1_adh_out[0]),
    .ADH1(const_gen_1_adh_out[1]), .ADH2(const_gen_1_adh_out[2]), .ADH3(const_gen_1_adh_out[3]),
    .ADH4(const_gen_1_adh_out[4]), .ADH5(const_gen_1_adh_out[5]), .ADH6(const_gen_1_adh_out[6]),
    .ADH7(const_gen_1_adh_out[7]), .PHI1(PHI1), .PHI2(PHI2));
  D_Flip_Flop #(.trigger("high")) d_ff_2 (.D(L_IRQ_ec2f2199), .clk(PHI2), .Qn(d_ff_2_qn));  // open: Q, preset, reset
  D_latch_6baf82dd irqp_latch (.NOT_Q(irqp_latch_not_q), .D(d_ff_2_qn), .EN(PHI1));  // open: Q
  Register #(.trigger("high")) X (.D(regs_1_x_debug), .en(1'b1), .clk(1'b1));  // open: Q, clr
  REGS regs_1 (
    .S_Debug(regs_1_s_debug), .out_19(regs_1_out_18[1]), .out_20(regs_1_out_18[2]), .SB3(regs_1_out_18[3]),
    .SB4(regs_1_out_18[4]), .SB5(regs_1_out_18[5]), .out_24(regs_1_out_18[6]), .out_25(regs_1_out_18[7]),
    .ADL0(regs_1_adl0[0]), .ADL1(regs_1_adl0[1]), .ADL2(regs_1_adl0[2]), .ADL3(regs_1_adl0[3]),
    .ADL4(regs_1_adl0[4]), .ADL5(regs_1_adl0[5]), .ADL6(regs_1_adl0[6]), .ADL7(regs_1_adl0[7]),
    .out_18(regs_1_out_18[0]), .Y_Debug(regs_1_y_debug), .X_Debug(regs_1_x_debug),
    .Y_SB_981fc62c(random_logic_1_y_sb_981fc62c[0]), .SB_Y_f952d371(random_logic_1_y_sb_981fc62c[1]),
    .X_SB_50e8fb84(random_logic_1_y_sb_981fc62c[2]), .SB_X_a4a389b1(random_logic_1_y_sb_981fc62c[3]),
    .S_ADL_299349f9(random_logic_1_y_sb_981fc62c[4]), .S_S_0e77937e(random_logic_1_y_sb_981fc62c[5]),
    .SB_S_e7e7b943(random_logic_1_y_sb_981fc62c[6]), .S_SB_c8f0deaa(random_logic_1_y_sb_981fc62c[7]),
    .SB0(precharge_1_sb_out[0]), .SB1(precharge_1_sb_out[1]), .SB2(precharge_1_sb_out[2]),
    .in_13(precharge_1_sb_out[3]), .in_14(precharge_1_sb_out[4]), .in_15(precharge_1_sb_out[5]),
    .SB6(precharge_1_sb_out[6]), .PHI2(PHI2), .SB7(precharge_1_sb_out[7]));
  Register #(.trigger("high")) Y (.D(regs_1_y_debug), .en(1'b1), .clk(1'b1));  // open: Q, clr
  Register #(.trigger("high")) S (.D(regs_1_s_debug), .en(1'b1), .clk(1'b1));  // open: Q, clr
  not not_2 (not_2_out, RDY);
  Register #(.trigger("high")) AI (.D(alu_1_ai_debug), .en(1'b1), .clk(1'b1));  // open: Q, clr
  D_latch_6baf82dd prdy_latch1 (.NOT_Q(prdy_latch1_not_q), .D(not_2_out), .EN(PHI2));  // open: Q
  ALU alu_1 (
    .out_55(regs_1_out_18[2]), .out_59(regs_1_out_18[3]), .SB4(regs_1_out_18[4]), .SB5(regs_1_out_18[5]),
    .SB6(regs_1_out_18[6]), .SB7(regs_1_out_18[7]), .SB0(regs_1_out_18[0]), .SB1(regs_1_out_18[1]),
    .DB2(random_logic_1_db0[2]), .out_60(random_logic_1_db0[3]), .DB4(random_logic_1_db0[4]),
    .out_68(random_logic_1_db0[5]), .DB6(random_logic_1_db0[6]), .DB7(random_logic_1_db0[7]),
    .DB0(random_logic_1_db0[0]), .out_52(random_logic_1_db0[1]), .ADL2(regs_1_adl0[2]),
    .ADL3(regs_1_adl0[3]), .ADL4(regs_1_adl0[4]), .ADL5(regs_1_adl0[5]), .ADL6(regs_1_adl0[6]),
    .ADL7(regs_1_adl0[7]), .ADL0(regs_1_adl0[0]), .ADL1(regs_1_adl0[1]), .AC_Debug(alu_1_ac_debug),
    .ADH2(alu_1_adh0[2]), .ADH3(alu_1_adh0[3]), .ADH4(alu_1_adh0[4]), .ADH5(alu_1_adh0[5]),
    .ADH6(alu_1_adh0[6]), .ADH7(alu_1_adh0[7]), .ADH0(alu_1_adh0[0]), .ADH1(alu_1_adh0[1]), .ACR(alu_1_acr),
    .AVR(alu_1_avr), .AI_Debug(alu_1_ai_debug), .BI_Debug(alu_1_bi_debug), .ADD_Debug(alu_1_add_debug),
    .SB2(precharge_1_sb_out[2]), .SB3(precharge_1_sb_out[3]), .in_33(precharge_1_sb_out[4]),
    .in_35(precharge_1_sb_out[5]), .in_37(precharge_1_sb_out[6]), .in_39(precharge_1_sb_out[7]),
    .NDB_ADD_5826378a(random_logic_1_ndb_add_5826378a[0]),
    .DB_ADD_49072aec(random_logic_1_ndb_add_5826378a[1]),
    .L_0_ADD_7d0d5e3b(random_logic_1_ndb_add_5826378a[2]),
    .SB_ADD_21cc08e7(random_logic_1_ndb_add_5826378a[3]),
    .ADL_ADD_b3e2e6b8(random_logic_1_ndb_add_5826378a[4]),
    .ADD_SB06_79b3146b(random_logic_1_ndb_add_5826378a[5]),
    .ADD_SB7_3b72c6f5(random_logic_1_ndb_add_5826378a[6]),
    .ADD_ADL_d25cdcd8(random_logic_1_ndb_add_5826378a[7]), .ANDS(random_logic_1_ndb_add_5826378a[8]),
    .EORS(random_logic_1_ndb_add_5826378a[9]), .ORS(random_logic_1_ndb_add_5826378a[10]),
    .SRS(random_logic_1_ndb_add_5826378a[11]), .SUMS(random_logic_1_ndb_add_5826378a[12]),
    .SB_AC_692b76aa(random_logic_1_sb_adh_3fc727a4[4]), .AC_SB_4f3a8e20(random_logic_1_sb_adh_3fc727a4[3]),
    .AC_DB_7461a43f(random_logic_1_sb_adh_3fc727a4[2]), .SB_DB_92ea0e91(random_logic_1_sb_adh_3fc727a4[1]),
    .PHI2(PHI2), .SB_ADH_3fc727a4(random_logic_1_sb_adh_3fc727a4[0]),
    .L_ACIN_e8912140(random_logic_1_l_acin_e8912140[0]), .L_DAA_9902be4a(random_logic_1_l_acin_e8912140[1]),
    .L_DSA_8e87f2a8(random_logic_1_l_acin_e8912140[2]), .in_23(precharge_1_sb_out[0]),
    .in_26(precharge_1_sb_out[1]), .in_30(precharge_1_db_out[2]), .DB3(precharge_1_db_out[3]),
    .in_34(precharge_1_db_out[4]), .DB5(precharge_1_db_out[5]), .in_38(precharge_1_db_out[6]),
    .in_40(precharge_1_db_out[7]), .in_24(precharge_1_db_out[0]), .DB1(precharge_1_db_out[1]),
    .ADL_In(const_gen_1_adl_out), .ADH_In(const_gen_1_adh_out));
  Register #(.trigger("high")) BI (.D(alu_1_bi_debug), .en(1'b1), .clk(1'b1));  // open: Q, clr
  D_latch_6baf82dd prdy_latch2 (.NOT_Q(prdy_latch2_not_q), .D(prdy_latch1_not_q), .EN(PHI1));  // open: Q
  Register #(.trigger("high")) ADD (.D(alu_1_add_debug), .en(1'b1), .clk(1'b1));  // open: Q, clr
  D_Flip_Flop #(.trigger("high")) d_ff_3 (.D(L_RES_2d8f5153), .clk(PHI2), .Q(d_ff_3_q));  // open: Qn, preset, reset
  Register #(.trigger("high")) AC (.D(alu_1_ac_debug), .en(1'b1), .clk(1'b1));  // open: Q, clr
  D_latch_6baf82dd resp_latch (.NOT_Q(resp_latch_not_q), .D(d_ff_3_q), .EN(PHI1));  // open: Q
  PC pc_1 (
    .DB2(random_logic_1_db0[2]), .DB3(random_logic_1_db0[3]), .DB4(random_logic_1_db0[4]),
    .DB5(random_logic_1_db0[5]), .DB6(random_logic_1_db0[6]), .DB7(random_logic_1_db0[7]),
    .ADL0(regs_1_adl0[0]), .out_36(regs_1_adl0[1]), .ADL2(regs_1_adl0[2]), .ADL3(regs_1_adl0[3]),
    .out_39(regs_1_adl0[4]), .out_40(regs_1_adl0[5]), .out_41(regs_1_adl0[6]), .DB0(random_logic_1_db0[0]),
    .ADL7(regs_1_adl0[7]), .out_43(alu_1_adh0[0]), .ADH1(alu_1_adh0[1]), .out_45(alu_1_adh0[2]),
    .out_46(alu_1_adh0[3]), .ADH4(alu_1_adh0[4]), .ADH5(alu_1_adh0[5]), .ADH6(alu_1_adh0[6]),
    .ADH7(alu_1_adh0[7]), .DB1(random_logic_1_db0[1]), .PC_Debug(pc_1_pc_debug), .PCS_Debug(pc_1_pcs_debug),
    .ADL_PCL_0d330abd(random_logic_1_adh_pch_413c8ef5[4]),
    .PCL_PCL_effd7227(random_logic_1_adh_pch_413c8ef5[5]),
    .PCL_ADL_75837bef(random_logic_1_adh_pch_413c8ef5[6]),
    .PCL_DB_8c5417e4(random_logic_1_adh_pch_413c8ef5[7]),
    .ADH_PCH_413c8ef5(random_logic_1_adh_pch_413c8ef5[0]),
    .PCH_PCH_e0d1ea0f(random_logic_1_adh_pch_413c8ef5[1]),
    .PCH_ADH_329c7fb7(random_logic_1_adh_pch_413c8ef5[2]),
    .PCH_DB_4d5eb992(random_logic_1_adh_pch_413c8ef5[3]),
    .L_1_PC_f7ea2184(random_logic_1_adh_pch_413c8ef5[8]), .PHI2(PHI2), .in_11(const_gen_1_adl_out[0]),
    .ADL1(const_gen_1_adl_out[1]), .in_13(const_gen_1_adl_out[2]), .in_14(const_gen_1_adl_out[3]),
    .ADL4(const_gen_1_adl_out[4]), .ADL5(const_gen_1_adl_out[5]), .ADL6(const_gen_1_adl_out[6]),
    .in_18(const_gen_1_adl_out[7]), .ADH0(const_gen_1_adh_out[0]), .in_20(const_gen_1_adh_out[1]),
    .ADH2(const_gen_1_adh_out[2]), .ADH3(const_gen_1_adh_out[3]), .in_23(const_gen_1_adh_out[4]),
    .in_24(const_gen_1_adh_out[5]), .in_25(const_gen_1_adh_out[6]), .in_26(const_gen_1_adh_out[7]));
  Register #(.trigger("high"), .width(16)) PC_2 (.D(pc_1_pc_debug), .en(1'b1), .clk(1'b1));  // open: Q, clr
  Register #(.trigger("high"), .width(16)) PCS (.D(pc_1_pcs_debug), .en(1'b1), .clk(1'b1));  // open: Q, clr
  CLOCKGEN clockgen_1 (.PHI2(PHI2), .PHI1(PHI1), .PHI0(PHI0));
  not not_3 (not_3_out, ir_1_ir5);
  DL dl_1 (
    .out_53(out_41), .D7(out_42), .DB2(random_logic_1_db0[2]), .DB3(random_logic_1_db0[3]),
    .out_27(random_logic_1_db0[4]), .DB5(random_logic_1_db0[5]), .out_29(random_logic_1_db0[6]),
    .DB7(random_logic_1_db0[7]), .ADL0(regs_1_adl0[0]), .ADL1(regs_1_adl0[1]), .ADL2(regs_1_adl0[2]),
    .ADL3(regs_1_adl0[3]), .ADL4(regs_1_adl0[4]), .ADL5(regs_1_adl0[5]), .ADL6(regs_1_adl0[6]),
    .ADL7(regs_1_adl0[7]), .ADH0(alu_1_adh0[0]), .DB0(random_logic_1_db0[0]), .ADH1(alu_1_adh0[1]),
    .ADH2(alu_1_adh0[2]), .ADH3(alu_1_adh0[3]), .ADH4(alu_1_adh0[4]), .ADH5(alu_1_adh0[5]),
    .ADH6(alu_1_adh0[6]), .ADH7(alu_1_adh0[7]), .out_47(out_27), .out_48(D1), .out_49(D2),
    .DB1(random_logic_1_db0[1]), .out_50(out_30), .out_51(out_31), .D5(D5), .DL_Debug(dl_1_dl_debug),
    .DOR_Debug(dl_1_dor_debug), .WR(random_logic_1_wr), .DL_ADL_73e48c13(random_logic_1_dl_adl_73e48c13[0]),
    .DL_ADH_067137e0(random_logic_1_dl_adl_73e48c13[2]), .DL_DB_4a6f16a8(random_logic_1_dl_adl_73e48c13[1]),
    .in_7(precharge_1_db_out[0]), .in_8(precharge_1_db_out[1]), .in_9(precharge_1_db_out[2]),
    .in_10(precharge_1_db_out[3]), .DB4(precharge_1_db_out[4]), .in_12(precharge_1_db_out[5]), .PHI1(PHI1),
    .DB6(precharge_1_db_out[6]), .in_14(precharge_1_db_out[7]), .D0(D0), .D1(in_8), .D2(in_9), .D3(D3),
    .D4(D4), .PHI2(PHI2), .in_20(in_12), .D6(D6), .in_22(D7));
  Register #(.trigger("high")) DL_2 (.D(dl_1_dl_debug), .en(1'b1), .clk(1'b1));  // open: Q, clr
  D_latch_6baf82dd RWLatch (.NOT_Q(R_W_0418701b), .D(random_logic_1_wr), .EN(PHI1));  // open: Q
  IR ir_1 (
    .IR0(ir_1_ir0), .IR1(ir_1_ir1), .IR2(ir_1_ir2), .IR3(ir_1_ir3), .IR4(ir_1_ir4), .IR5(ir_1_ir5),
    .IR6(ir_1_ir6), .IR7(ir_1_ir7), .FETCH(random_logic_1_fetch), .PHI1(PHI1),
    .L_in0_1c298b0d(predecode_1_l_pd0_72855f64), .L_in1_b96cc992(predecode_1_l_pd1_c99f14c8),
    .L_in2_3083e2d8(predecode_1_l_pd2_8bc41618), .L_in3_a5a5d143(predecode_1_l_pd3_ba6a24ea),
    .L_in4_0a50808c(predecode_1_l_pd4_9583460c), .L_in5_0608b880(predecode_1_l_pd5_8dc63d2b),
    .L_in6_2fe22dcd(predecode_1_l_pd6_87750ded), .L_in7_62f2dc0e(predecode_1_l_pd7_40cf097f));
  Register #(.trigger("high")) DOR (.D(dl_1_dor_debug), .en(1'b1), .clk(1'b1));  // open: Q, clr
  PREDECODE predecode_1 (
    .L_TWOCYCLE_43089fae(predecode_1_l_twocycle_43089fae),
    .L_IMPLIED_7f832bff(predecode_1_l_implied_7f832bff), .L_PD0_72855f64(predecode_1_l_pd0_72855f64),
    .L_PD1_c99f14c8(predecode_1_l_pd1_c99f14c8), .L_PD2_8bc41618(predecode_1_l_pd2_8bc41618),
    .L_PD3_ba6a24ea(predecode_1_l_pd3_ba6a24ea), .L_PD4_9583460c(predecode_1_l_pd4_9583460c),
    .L_PD5_8dc63d2b(predecode_1_l_pd5_8dc63d2b), .L_PD6_87750ded(predecode_1_l_pd6_87750ded),
    .L_PD7_40cf097f(predecode_1_l_pd7_40cf097f), .D0(D0), .D1(in_8), .D2(in_9), .PHI2(PHI2), .D3(D3),
    .D4(D4), .D5(in_12), .D6(D6), .D7(D7), .L_0_IR_fde7bd13(random_logic_1_l_0_ir_fde7bd13));

  // Notes on the sheet:
  //   PHI2
  //   PHI1
  //   PHI1
  //   PHI2
  //   T1
  //   The pin layout corresponds to the real chip
  //   /NMIP
  //   /IRQP
  //   ADH in/out
  //   ADL in/out
  //   DB in/out
  //   SB in/out
  //   DEBUG
  //   /PRDY
  //   DEBUG
  //   RESP
  //   DEBUG
  //   PHI2
  //   PHI1
  //   WR
  //   DEBUG
  //   PHI1
  //   PHI2
endmodule

module CLOCKGEN (
  input  PHI0,
  output PHI2,
  output PHI1
);

  wire not_1_out;

  not not_1 (not_1_out, PHI0);
  not not_2 (PHI1, PHI0);
  not not_3 (PHI2, not_1_out);
endmodule

module IR (
  input  FETCH,
  input  PHI1,
  input  L_in0_1c298b0d,
  input  L_in1_b96cc992,
  input  L_in2_3083e2d8,
  input  L_in3_a5a5d143,
  input  L_in4_0a50808c,
  input  L_in5_0608b880,
  input  L_in6_2fe22dcd,
  input  L_in7_62f2dc0e,
  output IR0,
  output IR1,
  output IR2,
  output IR3,
  output IR4,
  output IR5,
  output IR6,
  output IR7
);

  wire and1_out;

  and and1 (and1_out, FETCH, PHI1);
  D_latch_6baf82dd d_latch_6baf82dd_1 (.NOT_Q(IR0), .D(L_in0_1c298b0d), .EN(and1_out));  // open: Q
  D_latch_6baf82dd d_latch_6baf82dd_2 (.NOT_Q(IR1), .D(L_in1_b96cc992), .EN(and1_out));  // open: Q
  D_latch_6baf82dd d_latch_6baf82dd_3 (.NOT_Q(IR2), .D(L_in2_3083e2d8), .EN(and1_out));  // open: Q
  D_latch_6baf82dd d_latch_6baf82dd_4 (.NOT_Q(IR3), .D(L_in3_a5a5d143), .EN(and1_out));  // open: Q
  D_latch_6baf82dd d_latch_6baf82dd_5 (.NOT_Q(IR4), .D(L_in4_0a50808c), .EN(and1_out));  // open: Q
  D_latch_6baf82dd d_latch_6baf82dd_6 (.NOT_Q(IR5), .D(L_in5_0608b880), .EN(and1_out));  // open: Q
  D_latch_6baf82dd d_latch_6baf82dd_7 (.NOT_Q(IR6), .D(L_in6_2fe22dcd), .EN(and1_out));  // open: Q
  D_latch_6baf82dd d_latch_6baf82dd_8 (.NOT_Q(IR7), .D(L_in7_62f2dc0e), .EN(and1_out));  // open: Q
endmodule
// DECODER
module DECODER_TRANS (
  input  L_T5_e9d210fb,
  input  L_T4_1ff9fe8e,
  input  L_T3_2730c10f,
  input  L_T2_2b20ddce,
  input  IR0,
  input  IR1,
  input  IR7,
  input  IR4,
  input  IR3,
  input  IR2,
  input  IR6,
  input  IR5,
  input  L_T0_be2341f9,
  input  L_T1X_cd47d06e,
  output L_0_4ba6ff26,
  output L_1_3b22cb4c,
  output L_2_4a831fe0,
  output L_3_16a57085,
  output L_4_45284221,
  output L_5_79aea93e,
  output L_6_420976ce,
  output L_7_6f2638d9,
  output L_8_129a8ae9,
  output L_9_953a8f61,
  output L_10_6da465ad,
  output L_11_4ca67c7e,
  output L_12_142439c6,
  output L_13_20e8ba47,
  output L_14_5208a13d,
  output L_15_991215f6,
  output L_16_663400da,
  output L_17_d2862fba,
  output L_18_04a5e6fc,
  output L_19_7b271e4d,
  output L_20_8c61ee26,
  output L_21_feeca76b,
  output L_22_7a606cb8,
  output L_23_91cdc8b5,
  output L_24_62a90c42,
  output L_25_ec7c8b92,
  output L_26_4792594e,
  output L_27_bffb8973,
  output L_28_d2630233,
  output L_29_28b5b79d,
  output L_30_13bc78e9,
  output L_31_d65b4f16,
  output L_32_a76bc5d3,
  output L_33_4c80d111,
  output L_34_ec404986,
  output L_35_a3ad9e97,
  output L_36_f906ff59,
  output L_37_970560ea,
  output L_38_44e13d1d,
  output L_39_ab49266d,
  output L_40_b0ce7c4d,
  output L_41_5ba99609,
  output L_42_05de627d,
  output L_43_e53210b4,
  output L_44_7557d7f6,
  output L_45_d477530d,
  output L_46_8026585c,
  output L_47_50b9384c,
  output L_48_961f2eda,
  output L_49_b961b159,
  output L_50_7cd0b929,
  output L_51_73afc739,
  output L_52_6bbb5c5f,
  output L_53_db17dfc3,
  output L_54_df2d9682,
  output L_55_9656bee7,
  output L_56_ff4a974b,
  output L_57_bd139f3f,
  output L_58_b698ce08,
  output L_59_15390865,
  output L_60_ba37dadc,
  output L_61_aa3c3e0c,
  output L_62_1cf1b605,
  output L_63_0219edaa,
  output L_64_c9babf32,
  output L_65_a97300ad,
  output L_66_53023e8d,
  output L_67_07e7e8b6,
  output L_68_a93b1446,
  output L_69_c6a8c7bd,
  output L_70_14a93969,
  output L_71_037940dd,
  output L_72_65280ac2,
  output L_73_116545e2,
  output L_74_8a887fe0,
  output L_75_fbc631d3,
  output L_76_0c9e8790,
  output L_77_8a8d3736,
  output L_78_142fff2c,
  output L_79_88caeb61,
  output L_80_442d40a3,
  output L_81_7ac19b4f,
  output L_82_53fd2612,
  output L_83_8900340a,
  output L_84_4e42f7b7,
  output L_85_90e036dc,
  output L_86_fae89fad,
  output L_87_be04a52b,
  output L_88_ae4b2cef,
  output L_89_f62eed49,
  output L_90_d21e06c7,
  output L_91_1b0c0c3e,
  output L_92_0642b8ec,
  output L_93_66c1bc08,
  output L_94_c36cbd45,
  output L_95_8b08e919,
  output L_96_4be017a7,
  output L_97_91c265e2,
  output L_98_1dfb9b6f,
  output L_99_0cc83ca0,
  output L_100_35836628,
  output L_101_9d393967,
  output L_102_881ca15e,
  output L_103_46ba03e4,
  output L_104_2077d36b,
  output L_105_a29cdf8d,
  output L_106_36001eab,
  output L_107_68d37105,
  output L_108_a15fa495,
  output L_109_8b0ee0a1,
  output L_110_e7c60ed0,
  output L_111_1042ad89,
  output L_112_063f5ab4,
  output L_113_69d8438b,
  output L_114_a7bf33c8,
  output L_115_0ffd4dd7,
  output L_116_f87463c5,
  output L_117_54ea7dab,
  output L_118_25ed7443,
  output L_119_bc2ca239,
  output L_120_bf62daef,
  output L_121_348bd5c4,
  output L_122_2b9e98b2,
  output L_123_ea048c49,
  output L_124_3cfed9ae,
  output L_125_0b8e34b8,
  output L_126_b55b24f6,
  output L_127_f6767dc7,
  output L_128_aad3a25e,
  output L_129_8838ebbd
);

  wire not_1_out, not_2_out, not_3_out, not_4_out, not_5_out, not_6_out, not_7_out, not_8_out, or_1_out;

  not not_1 (not_1_out, IR1);
  or or_1 (or_1_out, IR0, IR1);
  not not_2 (not_2_out, IR0);
  not not_3 (not_3_out, IR7);
  not not_4 (not_4_out, IR4);
  not not_5 (not_5_out, IR3);
  not not_6 (not_6_out, IR2);
  not not_7 (not_7_out, IR6);
  not not_8 (not_8_out, IR5);
  Pull_Resistor #(.pull(1)) pull_resistor_1 (.node(L_0_4ba6ff26));
  Pull_Resistor #(.pull(1)) pull_resistor_2 (.node(L_1_3b22cb4c));
  Transistor #(.\type ("n")) transistor_1 (.in(1'b0), .out(L_1_3b22cb4c), .gate(L_T3_2730c10f));
  Transistor #(.\type ("n")) transistor_2 (.in(1'b0), .out(L_0_4ba6ff26), .gate(or_1_out));
  Transistor #(.\type ("n")) transistor_3 (.in(1'b0), .out(L_1_3b22cb4c), .gate(not_2_out));
  Transistor #(.\type ("n")) transistor_4 (.in(1'b0), .out(L_0_4ba6ff26), .gate(not_3_out));
  Transistor #(.\type ("n")) transistor_5 (.in(1'b0), .out(L_0_4ba6ff26), .gate(not_4_out));
  Transistor #(.\type ("n")) transistor_6 (.in(1'b0), .out(L_1_3b22cb4c), .gate(not_4_out));
  Transistor #(.\type ("n")) transistor_7 (.in(1'b0), .out(L_1_3b22cb4c), .gate(IR3));
  Transistor #(.\type ("n")) transistor_8 (.in(1'b0), .out(L_1_3b22cb4c), .gate(IR2));
  Transistor #(.\type ("n")) transistor_9 (.in(1'b0), .out(L_0_4ba6ff26), .gate(not_6_out));
  Transistor #(.\type ("n")) transistor_10 (.in(1'b0), .out(L_0_4ba6ff26), .gate(IR6));
  Transistor #(.\type ("n")) transistor_11 (.in(1'b0), .out(L_0_4ba6ff26), .gate(IR5));
  Pull_Resistor #(.pull(1)) pull_resistor_3 (.node(L_2_4a831fe0));
  Transistor #(.\type ("n")) transistor_12 (.in(1'b0), .out(L_2_4a831fe0), .gate(L_T2_2b20ddce));
  Transistor #(.\type ("n")) transistor_13 (.in(1'b0), .out(L_2_4a831fe0), .gate(not_2_out));
  Transistor #(.\type ("n")) transistor_14 (.in(1'b0), .out(L_2_4a831fe0), .gate(not_4_out));
  Transistor #(.\type ("n")) transistor_15 (.in(1'b0), .out(L_2_4a831fe0), .gate(not_5_out));
  Transistor #(.\type ("n")) transistor_16 (.in(1'b0), .out(L_2_4a831fe0), .gate(IR2));
  Pull_Resistor #(.pull(1)) pull_resistor_4 (.node(L_3_16a57085));
  Transistor #(.\type ("n")) transistor_17 (.in(1'b0), .out(L_3_16a57085), .gate(or_1_out));
  Transistor #(.\type ("n")) transistor_18 (.in(1'b0), .out(L_3_16a57085), .gate(not_3_out));
  Transistor #(.\type ("n")) transistor_19 (.in(1'b0), .out(L_3_16a57085), .gate(IR4));
  Transistor #(.\type ("n")) transistor_20 (.in(1'b0), .out(L_3_16a57085), .gate(not_5_out));
  Transistor #(.\type ("n")) transistor_21 (.in(1'b0), .out(L_3_16a57085), .gate(IR2));
  Transistor #(.\type ("n")) transistor_22 (.in(1'b0), .out(L_3_16a57085), .gate(IR5));
  Transistor #(.\type ("n")) transistor_23 (.in(1'b0), .out(L_3_16a57085), .gate(L_T0_be2341f9));
  Pull_Resistor #(.pull(1)) pull_resistor_5 (.node(L_4_45284221));
  Pull_Resistor #(.pull(1)) pull_resistor_6 (.node(L_5_79aea93e));
  Transistor #(.\type ("n")) transistor_24 (.in(1'b0), .out(L_4_45284221), .gate(or_1_out));
  Transistor #(.\type ("n")) transistor_25 (.in(1'b0), .out(L_5_79aea93e), .gate(or_1_out));
  Transistor #(.\type ("n")) transistor_26 (.in(1'b0), .out(L_4_45284221), .gate(not_3_out));
  Transistor #(.\type ("n")) transistor_27 (.in(1'b0), .out(L_5_79aea93e), .gate(not_3_out));
  Transistor #(.\type ("n")) transistor_28 (.in(1'b0), .out(L_5_79aea93e), .gate(IR4));
  Transistor #(.\type ("n")) transistor_29 (.in(1'b0), .out(L_4_45284221), .gate(not_4_out));
  Transistor #(.\type ("n")) transistor_30 (.in(1'b0), .out(L_4_45284221), .gate(not_5_out));
  Transistor #(.\type ("n")) transistor_31 (.in(1'b0), .out(L_4_45284221), .gate(IR2));
  Transistor #(.\type ("n")) transistor_32 (.in(1'b0), .out(L_4_45284221), .gate(IR6));
  Transistor #(.\type ("n")) transistor_33 (.in(1'b0), .out(L_5_79aea93e), .gate(not_7_out));
  Transistor #(.\type ("n")) transistor_34 (.in(1'b0), .out(L_4_45284221), .gate(IR5));
  Transistor #(.\type ("n")) transistor_35 (.in(1'b0), .out(L_5_79aea93e), .gate(IR5));
  Transistor #(.\type ("n")) transistor_36 (.in(1'b0), .out(L_4_45284221), .gate(L_T0_be2341f9));
  Transistor #(.\type ("n")) transistor_37 (.in(1'b0), .out(L_5_79aea93e), .gate(L_T0_be2341f9));
  Pull_Resistor #(.pull(1)) pull_resistor_7 (.node(L_6_420976ce));
  Transistor #(.\type ("n")) transistor_38 (.in(1'b0), .out(L_6_420976ce), .gate(L_T2_2b20ddce));
  Transistor #(.\type ("n")) transistor_39 (.in(1'b0), .out(L_6_420976ce), .gate(not_4_out));
  Transistor #(.\type ("n")) transistor_40 (.in(1'b0), .out(L_6_420976ce), .gate(not_6_out));
  Pull_Resistor #(.pull(1)) pull_resistor_8 (.node(L_7_6f2638d9));
  Transistor #(.\type ("n")) transistor_41 (.in(1'b0), .out(L_7_6f2638d9), .gate(not_1_out));
  Transistor #(.\type ("n")) transistor_42 (.in(1'b0), .out(L_7_6f2638d9), .gate(not_3_out));
  Transistor #(.\type ("n")) transistor_43 (.in(1'b0), .out(L_7_6f2638d9), .gate(IR6));
  Pull_Resistor #(.pull(1)) pull_resistor_9 (.node(L_8_129a8ae9));
  Pull_Resistor #(.pull(1)) pull_resistor_10 (.node(L_9_953a8f61));
  Transistor #(.\type ("n")) transistor_44 (.in(1'b0), .out(L_8_129a8ae9), .gate(L_T2_2b20ddce));
  Transistor #(.\type ("n")) transistor_45 (.in(1'b0), .out(L_9_953a8f61), .gate(not_1_out));
  Transistor #(.\type ("n")) transistor_46 (.in(1'b0), .out(L_8_129a8ae9), .gate(not_2_out));
  Transistor #(.\type ("n")) transistor_47 (.in(1'b0), .out(L_9_953a8f61), .gate(not_3_out));
  Transistor #(.\type ("n")) transistor_48 (.in(1'b0), .out(L_8_129a8ae9), .gate(IR4));
  Transistor #(.\type ("n")) transistor_49 (.in(1'b0), .out(L_9_953a8f61), .gate(IR4));
  Transistor #(.\type ("n")) transistor_50 (.in(1'b0), .out(L_8_129a8ae9), .gate(IR3));
  Transistor #(.\type ("n")) transistor_51 (.in(1'b0), .out(L_9_953a8f61), .gate(not_5_out));
  Transistor #(.\type ("n")) transistor_52 (.in(1'b0), .out(L_8_129a8ae9), .gate(IR2));
  Transistor #(.\type ("n")) transistor_53 (.in(1'b0), .out(L_9_953a8f61), .gate(IR2));
  Transistor #(.\type ("n")) transistor_54 (.in(1'b0), .out(L_9_953a8f61), .gate(IR6));
  Transistor #(.\type ("n")) transistor_55 (.in(1'b0), .out(L_9_953a8f61), .gate(IR5));
  Transistor #(.\type ("n")) transistor_56 (.in(1'b0), .out(L_9_953a8f61), .gate(L_T0_be2341f9));
  Pull_Resistor #(.pull(1)) pull_resistor_11 (.node(L_10_6da465ad));
  Transistor #(.\type ("n")) transistor_57 (.in(1'b0), .out(L_10_6da465ad), .gate(not_1_out));
  Transistor #(.\type ("n")) transistor_58 (.in(1'b0), .out(L_10_6da465ad), .gate(not_3_out));
  Transistor #(.\type ("n")) transistor_59 (.in(1'b0), .out(L_10_6da465ad), .gate(IR4));
  Transistor #(.\type ("n")) transistor_60 (.in(1'b0), .out(L_10_6da465ad), .gate(not_5_out));
  Transistor #(.\type ("n")) transistor_61 (.in(1'b0), .out(L_10_6da465ad), .gate(IR2));
  Transistor #(.\type ("n")) transistor_62 (.in(1'b0), .out(L_10_6da465ad), .gate(not_7_out));
  Transistor #(.\type ("n")) transistor_63 (.in(1'b0), .out(L_10_6da465ad), .gate(IR5));
  Transistor #(.\type ("n")) transistor_64 (.in(1'b0), .out(L_10_6da465ad), .gate(L_T0_be2341f9));
  Pull_Resistor #(.pull(1)) pull_resistor_12 (.node(L_11_4ca67c7e));
  Transistor #(.\type ("n")) transistor_65 (.in(1'b0), .out(L_11_4ca67c7e), .gate(or_1_out));
  Transistor #(.\type ("n")) transistor_66 (.in(1'b0), .out(L_11_4ca67c7e), .gate(not_3_out));
  Transistor #(.\type ("n")) transistor_67 (.in(1'b0), .out(L_11_4ca67c7e), .gate(IR4));
  Transistor #(.\type ("n")) transistor_68 (.in(1'b0), .out(L_11_4ca67c7e), .gate(not_7_out));
  Transistor #(.\type ("n")) transistor_69 (.in(1'b0), .out(L_11_4ca67c7e), .gate(not_8_out));
  Transistor #(.\type ("n")) transistor_70 (.in(1'b0), .out(L_11_4ca67c7e), .gate(L_T0_be2341f9));
  Pull_Resistor #(.pull(1)) pull_resistor_13 (.node(L_12_142439c6));
  Pull_Resistor #(.pull(1)) pull_resistor_14 (.node(L_13_20e8ba47));
  Transistor #(.\type ("n")) transistor_71 (.in(1'b0), .out(L_12_142439c6), .gate(not_1_out));
  Transistor #(.\type ("n")) transistor_72 (.in(1'b0), .out(L_13_20e8ba47), .gate(not_1_out));
  Transistor #(.\type ("n")) transistor_73 (.in(1'b0), .out(L_12_142439c6), .gate(not_3_out));
  Transistor #(.\type ("n")) transistor_74 (.in(1'b0), .out(L_13_20e8ba47), .gate(not_3_out));
  Transistor #(.\type ("n")) transistor_75 (.in(1'b0), .out(L_13_20e8ba47), .gate(not_4_out));
  Transistor #(.\type ("n")) transistor_76 (.in(1'b0), .out(L_13_20e8ba47), .gate(not_5_out));
  Transistor #(.\type ("n")) transistor_77 (.in(1'b0), .out(L_13_20e8ba47), .gate(IR2));
  Transistor #(.\type ("n")) transistor_78 (.in(1'b0), .out(L_12_142439c6), .gate(IR6));
  Transistor #(.\type ("n")) transistor_79 (.in(1'b0), .out(L_13_20e8ba47), .gate(IR6));
  Transistor #(.\type ("n")) transistor_80 (.in(1'b0), .out(L_12_142439c6), .gate(IR5));
  Transistor #(.\type ("n")) transistor_81 (.in(1'b0), .out(L_13_20e8ba47), .gate(IR5));
  Transistor #(.\type ("n")) transistor_82 (.in(1'b0), .out(L_13_20e8ba47), .gate(L_T0_be2341f9));
  Pull_Resistor #(.pull(1)) pull_resistor_15 (.node(L_14_5208a13d));
  Transistor #(.\type ("n")) transistor_83 (.in(1'b0), .out(L_14_5208a13d), .gate(not_1_out));
  Transistor #(.\type ("n")) transistor_84 (.in(1'b0), .out(L_14_5208a13d), .gate(not_3_out));
  Transistor #(.\type ("n")) transistor_85 (.in(1'b0), .out(L_14_5208a13d), .gate(IR6));
  Transistor #(.\type ("n")) transistor_86 (.in(1'b0), .out(L_14_5208a13d), .gate(not_8_out));
  Transistor #(.\type ("n")) transistor_87 (.in(1'b0), .out(L_14_5208a13d), .gate(L_T0_be2341f9));
  Pull_Resistor #(.pull(1)) pull_resistor_16 (.node(L_15_991215f6));
  Transistor #(.\type ("n")) transistor_88 (.in(1'b0), .out(L_15_991215f6), .gate(not_1_out));
  Transistor #(.\type ("n")) transistor_89 (.in(1'b0), .out(L_15_991215f6), .gate(not_3_out));
  Transistor #(.\type ("n")) transistor_90 (.in(1'b0), .out(L_15_991215f6), .gate(IR4));
  Transistor #(.\type ("n")) transistor_91 (.in(1'b0), .out(L_15_991215f6), .gate(not_5_out));
  Transistor #(.\type ("n")) transistor_92 (.in(1'b0), .out(L_15_991215f6), .gate(IR2));
  Transistor #(.\type ("n")) transistor_93 (.in(1'b0), .out(L_15_991215f6), .gate(not_7_out));
  Transistor #(.\type ("n")) transistor_94 (.in(1'b0), .out(L_15_991215f6), .gate(IR5));
  Transistor #(.\type ("n")) transistor_95 (.in(1'b0), .out(L_15_991215f6), .gate(L_T1X_cd47d06e));
  Pull_Resistor #(.pull(1)) pull_resistor_17 (.node(L_16_663400da));
  Pull_Resistor #(.pull(1)) pull_resistor_18 (.node(L_17_d2862fba));
  Transistor #(.\type ("n")) transistor_96 (.in(1'b0), .out(L_17_d2862fba), .gate(not_1_out));
  Transistor #(.\type ("n")) transistor_97 (.in(1'b0), .out(L_16_663400da), .gate(or_1_out));
  Transistor #(.\type ("n")) transistor_98 (.in(1'b0), .out(L_16_663400da), .gate(not_3_out));
  Transistor #(.\type ("n")) transistor_99 (.in(1'b0), .out(L_17_d2862fba), .gate(not_3_out));
  Transistor #(.\type ("n")) transistor_100 (.in(1'b0), .out(L_16_663400da), .gate(IR4));
  Transistor #(.\type ("n")) transistor_101 (.in(1'b0), .out(L_17_d2862fba), .gate(not_4_out));
  Transistor #(.\type ("n")) transistor_102 (.in(1'b0), .out(L_16_663400da), .gate(not_5_out));
  Transistor #(.\type ("n")) transistor_103 (.in(1'b0), .out(L_17_d2862fba), .gate(not_5_out));
  Transistor #(.\type ("n")) transistor_104 (.in(1'b0), .out(L_16_663400da), .gate(IR2));
  Transistor #(.\type ("n")) transistor_105 (.in(1'b0), .out(L_17_d2862fba), .gate(IR2));
  Transistor #(.\type ("n")) transistor_106 (.in(1'b0), .out(L_17_d2862fba), .gate(IR6));
  Transistor #(.\type ("n")) transistor_107 (.in(1'b0), .out(L_16_663400da), .gate(not_7_out));
  Transistor #(.\type ("n")) transistor_108 (.in(1'b0), .out(L_16_663400da), .gate(not_8_out));
  Transistor #(.\type ("n")) transistor_109 (.in(1'b0), .out(L_17_d2862fba), .gate(not_8_out));
  Transistor #(.\type ("n")) transistor_110 (.in(1'b0), .out(L_17_d2862fba), .gate(L_T0_be2341f9));
  Transistor #(.\type ("n")) transistor_111 (.in(1'b0), .out(L_16_663400da), .gate(L_T1X_cd47d06e));
  Pull_Resistor #(.pull(1)) pull_resistor_19 (.node(L_18_04a5e6fc));
  Transistor #(.\type ("n")) transistor_112 (.in(1'b0), .out(L_18_04a5e6fc), .gate(or_1_out));
  Transistor #(.\type ("n")) transistor_113 (.in(1'b0), .out(L_18_04a5e6fc), .gate(not_3_out));
  Transistor #(.\type ("n")) transistor_114 (.in(1'b0), .out(L_18_04a5e6fc), .gate(IR4));
  Transistor #(.\type ("n")) transistor_115 (.in(1'b0), .out(L_18_04a5e6fc), .gate(not_5_out));
  Transistor #(.\type ("n")) transistor_116 (.in(1'b0), .out(L_18_04a5e6fc), .gate(IR2));
  Transistor #(.\type ("n")) transistor_117 (.in(1'b0), .out(L_18_04a5e6fc), .gate(IR5));
  Transistor #(.\type ("n")) transistor_118 (.in(1'b0), .out(L_18_04a5e6fc), .gate(L_T1X_cd47d06e));
  Pull_Resistor #(.pull(1)) pull_resistor_20 (.node(L_19_7b271e4d));
  Transistor #(.\type ("n")) transistor_119 (.in(1'b0), .out(L_19_7b271e4d), .gate(or_1_out));
  Transistor #(.\type ("n")) transistor_120 (.in(1'b0), .out(L_19_7b271e4d), .gate(not_3_out));
  Transistor #(.\type ("n")) transistor_121 (.in(1'b0), .out(L_19_7b271e4d), .gate(not_6_out));
  Transistor #(.\type ("n")) transistor_122 (.in(1'b0), .out(L_19_7b271e4d), .gate(IR6));
  Transistor #(.\type ("n")) transistor_123 (.in(1'b0), .out(L_19_7b271e4d), .gate(not_8_out));
  Transistor #(.\type ("n")) transistor_124 (.in(1'b0), .out(L_19_7b271e4d), .gate(L_T0_be2341f9));
  Pull_Resistor #(.pull(1)) pull_resistor_21 (.node(L_20_8c61ee26));
  Transistor #(.\type ("n")) transistor_125 (.in(1'b0), .out(L_20_8c61ee26), .gate(or_1_out));
  Transistor #(.\type ("n")) transistor_126 (.in(1'b0), .out(L_20_8c61ee26), .gate(not_3_out));
  Transistor #(.\type ("n")) transistor_127 (.in(1'b0), .out(L_20_8c61ee26), .gate(IR4));
  Transistor #(.\type ("n")) transistor_128 (.in(1'b0), .out(L_20_8c61ee26), .gate(IR6));
  Transistor #(.\type ("n")) transistor_129 (.in(1'b0), .out(L_20_8c61ee26), .gate(not_8_out));
  Transistor #(.\type ("n")) transistor_130 (.in(1'b0), .out(L_20_8c61ee26), .gate(L_T0_be2341f9));
  Pull_Resistor #(.pull(1)) pull_resistor_22 (.node(L_21_feeca76b));
  Transistor #(.\type ("n")) transistor_131 (.in(1'b0), .out(L_21_feeca76b), .gate(or_1_out));
  Transistor #(.\type ("n")) transistor_132 (.in(1'b0), .out(L_21_feeca76b), .gate(IR7));
  Transistor #(.\type ("n")) transistor_133 (.in(1'b0), .out(L_21_feeca76b), .gate(IR4));
  Transistor #(.\type ("n")) transistor_134 (.in(1'b0), .out(L_21_feeca76b), .gate(IR3));
  Transistor #(.\type ("n")) transistor_135 (.in(1'b0), .out(L_21_feeca76b), .gate(IR2));
  Transistor #(.\type ("n")) transistor_136 (.in(1'b0), .out(L_21_feeca76b), .gate(IR6));
  Transistor #(.\type ("n")) transistor_137 (.in(1'b0), .out(L_21_feeca76b), .gate(not_8_out));
  Transistor #(.\type ("n")) transistor_138 (.in(1'b0), .out(L_21_feeca76b), .gate(L_T0_be2341f9));
  Pull_Resistor #(.pull(1)) pull_resistor_23 (.node(L_22_7a606cb8));
  Transistor #(.\type ("n")) transistor_139 (.in(1'b0), .out(L_22_7a606cb8), .gate(L_T5_e9d210fb));
  Transistor #(.\type ("n")) transistor_140 (.in(1'b0), .out(L_22_7a606cb8), .gate(or_1_out));
  Transistor #(.\type ("n")) transistor_141 (.in(1'b0), .out(L_22_7a606cb8), .gate(IR7));
  Transistor #(.\type ("n")) transistor_142 (.in(1'b0), .out(L_22_7a606cb8), .gate(IR4));
  Transistor #(.\type ("n")) transistor_143 (.in(1'b0), .out(L_22_7a606cb8), .gate(IR3));
  Transistor #(.\type ("n")) transistor_144 (.in(1'b0), .out(L_22_7a606cb8), .gate(IR2));
  Transistor #(.\type ("n")) transistor_145 (.in(1'b0), .out(L_22_7a606cb8), .gate(IR6));
  Transistor #(.\type ("n")) transistor_146 (.in(1'b0), .out(L_22_7a606cb8), .gate(IR5));
  Pull_Resistor #(.pull(1)) pull_resistor_24 (.node(L_23_91cdc8b5));
  Transistor #(.\type ("n")) transistor_147 (.in(1'b0), .out(L_23_91cdc8b5), .gate(or_1_out));
  Transistor #(.\type ("n")) transistor_148 (.in(1'b0), .out(L_23_91cdc8b5), .gate(IR7));
  Transistor #(.\type ("n")) transistor_149 (.in(1'b0), .out(L_23_91cdc8b5), .gate(IR4));
  Transistor #(.\type ("n")) transistor_150 (.in(1'b0), .out(L_23_91cdc8b5), .gate(not_5_out));
  Transistor #(.\type ("n")) transistor_151 (.in(1'b0), .out(L_23_91cdc8b5), .gate(IR2));
  Transistor #(.\type ("n")) transistor_152 (.in(1'b0), .out(L_23_91cdc8b5), .gate(IR5));
  Transistor #(.\type ("n")) transistor_153 (.in(1'b0), .out(L_23_91cdc8b5), .gate(L_T0_be2341f9));
  Pull_Resistor #(.pull(1)) pull_resistor_25 (.node(L_24_62a90c42));
  Pull_Resistor #(.pull(1)) pull_resistor_26 (.node(L_25_ec7c8b92));
  Transistor #(.\type ("n")) transistor_154 (.in(1'b0), .out(L_24_62a90c42), .gate(L_T4_1ff9fe8e));
  Transistor #(.\type ("n")) transistor_155 (.in(1'b0), .out(L_25_ec7c8b92), .gate(L_T3_2730c10f));
  Transistor #(.\type ("n")) transistor_156 (.in(1'b0), .out(L_24_62a90c42), .gate(or_1_out));
  Transistor #(.\type ("n")) transistor_157 (.in(1'b0), .out(L_25_ec7c8b92), .gate(or_1_out));
  Transistor #(.\type ("n")) transistor_158 (.in(1'b0), .out(L_24_62a90c42), .gate(IR7));
  Transistor #(.\type ("n")) transistor_159 (.in(1'b0), .out(L_25_ec7c8b92), .gate(IR7));
  Transistor #(.\type ("n")) transistor_160 (.in(1'b0), .out(L_24_62a90c42), .gate(IR4));
  Transistor #(.\type ("n")) transistor_161 (.in(1'b0), .out(L_25_ec7c8b92), .gate(IR4));
  Transistor #(.\type ("n")) transistor_162 (.in(1'b0), .out(L_24_62a90c42), .gate(IR3));
  Transistor #(.\type ("n")) transistor_163 (.in(1'b0), .out(L_25_ec7c8b92), .gate(not_5_out));
  Transistor #(.\type ("n")) transistor_164 (.in(1'b0), .out(L_24_62a90c42), .gate(IR2));
  Transistor #(.\type ("n")) transistor_165 (.in(1'b0), .out(L_25_ec7c8b92), .gate(IR2));
  Transistor #(.\type ("n")) transistor_166 (.in(1'b0), .out(L_24_62a90c42), .gate(not_7_out));
  Transistor #(.\type ("n")) transistor_167 (.in(1'b0), .out(L_24_62a90c42), .gate(not_8_out));
  Transistor #(.\type ("n")) transistor_168 (.in(1'b0), .out(L_25_ec7c8b92), .gate(not_8_out));
  Pull_Resistor #(.pull(1)) pull_resistor_27 (.node(L_26_4792594e));
  Transistor #(.\type ("n")) transistor_169 (.in(1'b0), .out(L_26_4792594e), .gate(L_T5_e9d210fb));
  Transistor #(.\type ("n")) transistor_170 (.in(1'b0), .out(L_26_4792594e), .gate(or_1_out));
  Transistor #(.\type ("n")) transistor_171 (.in(1'b0), .out(L_26_4792594e), .gate(IR7));
  Transistor #(.\type ("n")) transistor_172 (.in(1'b0), .out(L_26_4792594e), .gate(IR4));
  Transistor #(.\type ("n")) transistor_173 (.in(1'b0), .out(L_26_4792594e), .gate(IR3));
  Transistor #(.\type ("n")) transistor_174 (.in(1'b0), .out(L_26_4792594e), .gate(IR2));
  Transistor #(.\type ("n")) transistor_175 (.in(1'b0), .out(L_26_4792594e), .gate(not_7_out));
  Transistor #(.\type ("n")) transistor_176 (.in(1'b0), .out(L_26_4792594e), .gate(IR5));
  Pull_Resistor #(.pull(1)) pull_resistor_28 (.node(L_27_bffb8973));
  Transistor #(.\type ("n")) transistor_177 (.in(1'b0), .out(L_27_bffb8973), .gate(not_1_out));
  Transistor #(.\type ("n")) transistor_178 (.in(1'b0), .out(L_27_bffb8973), .gate(IR7));
  Transistor #(.\type ("n")) transistor_179 (.in(1'b0), .out(L_27_bffb8973), .gate(not_7_out));
  Transistor #(.\type ("n")) transistor_180 (.in(1'b0), .out(L_27_bffb8973), .gate(not_8_out));
  Pull_Resistor #(.pull(1)) pull_resistor_29 (.node(L_28_d2630233));
  Pull_Resistor #(.pull(1)) pull_resistor_30 (.node(L_29_28b5b79d));
  Transistor #(.\type ("n")) transistor_181 (.in(1'b0), .out(L_28_d2630233), .gate(L_T2_2b20ddce));
  Transistor #(.\type ("n")) transistor_182 (.in(1'b0), .out(L_29_28b5b79d), .gate(not_2_out));
  Transistor #(.\type ("n")) transistor_183 (.in(1'b0), .out(L_29_28b5b79d), .gate(IR7));
  Transistor #(.\type ("n")) transistor_184 (.in(1'b0), .out(L_29_28b5b79d), .gate(not_7_out));
  Transistor #(.\type ("n")) transistor_185 (.in(1'b0), .out(L_29_28b5b79d), .gate(IR5));
  Transistor #(.\type ("n")) transistor_186 (.in(1'b0), .out(L_29_28b5b79d), .gate(L_T0_be2341f9));
  Pull_Resistor #(.pull(1)) pull_resistor_31 (.node(L_30_13bc78e9));
  Transistor #(.\type ("n")) transistor_187 (.in(1'b0), .out(L_30_13bc78e9), .gate(or_1_out));
  Transistor #(.\type ("n")) transistor_188 (.in(1'b0), .out(L_30_13bc78e9), .gate(IR7));
  Transistor #(.\type ("n")) transistor_189 (.in(1'b0), .out(L_30_13bc78e9), .gate(IR4));
  Transistor #(.\type ("n")) transistor_190 (.in(1'b0), .out(L_30_13bc78e9), .gate(not_5_out));
  Transistor #(.\type ("n")) transistor_191 (.in(1'b0), .out(L_30_13bc78e9), .gate(not_6_out));
  Transistor #(.\type ("n")) transistor_192 (.in(1'b0), .out(L_30_13bc78e9), .gate(not_7_out));
  Pull_Resistor #(.pull(1)) pull_resistor_32 (.node(L_31_d65b4f16));
  Transistor #(.\type ("n")) transistor_193 (.in(1'b0), .out(L_31_d65b4f16), .gate(L_T2_2b20ddce));
  Transistor #(.\type ("n")) transistor_194 (.in(1'b0), .out(L_31_d65b4f16), .gate(IR4));
  Transistor #(.\type ("n")) transistor_195 (.in(1'b0), .out(L_31_d65b4f16), .gate(not_5_out));
  Transistor #(.\type ("n")) transistor_196 (.in(1'b0), .out(L_31_d65b4f16), .gate(not_6_out));
  Pull_Resistor #(.pull(1)) pull_resistor_33 (.node(L_32_a76bc5d3));
  Pull_Resistor #(.pull(1)) pull_resistor_34 (.node(L_33_4c80d111));
  Transistor #(.\type ("n")) transistor_197 (.in(1'b0), .out(L_33_4c80d111), .gate(L_T2_2b20ddce));
  Transistor #(.\type ("n")) transistor_198 (.in(1'b0), .out(L_32_a76bc5d3), .gate(not_2_out));
  Transistor #(.\type ("n")) transistor_199 (.in(1'b0), .out(L_32_a76bc5d3), .gate(IR7));
  Transistor #(.\type ("n")) transistor_200 (.in(1'b0), .out(L_33_4c80d111), .gate(IR3));
  Transistor #(.\type ("n")) transistor_201 (.in(1'b0), .out(L_32_a76bc5d3), .gate(IR6));
  Transistor #(.\type ("n")) transistor_202 (.in(1'b0), .out(L_32_a76bc5d3), .gate(IR5));
  Transistor #(.\type ("n")) transistor_203 (.in(1'b0), .out(L_32_a76bc5d3), .gate(L_T0_be2341f9));
  Pull_Resistor #(.pull(1)) pull_resistor_35 (.node(L_34_ec404986));
  Transistor #(.\type ("n")) transistor_204 (.in(1'b0), .out(L_34_ec404986), .gate(L_T0_be2341f9));
  Pull_Resistor #(.pull(1)) pull_resistor_36 (.node(L_35_a3ad9e97));
  Transistor #(.\type ("n")) transistor_205 (.in(1'b0), .out(L_35_a3ad9e97), .gate(L_T2_2b20ddce));
  Transistor #(.\type ("n")) transistor_206 (.in(1'b0), .out(L_35_a3ad9e97), .gate(or_1_out));
  Transistor #(.\type ("n")) transistor_207 (.in(1'b0), .out(L_35_a3ad9e97), .gate(IR7));
  Transistor #(.\type ("n")) transistor_208 (.in(1'b0), .out(L_35_a3ad9e97), .gate(IR4));
  Transistor #(.\type ("n")) transistor_209 (.in(1'b0), .out(L_35_a3ad9e97), .gate(IR2));
  Pull_Resistor #(.pull(1)) pull_resistor_37 (.node(L_36_f906ff59));
  Transistor #(.\type ("n")) transistor_210 (.in(1'b0), .out(L_36_f906ff59), .gate(L_T3_2730c10f));
  Transistor #(.\type ("n")) transistor_211 (.in(1'b0), .out(L_36_f906ff59), .gate(or_1_out));
  Transistor #(.\type ("n")) transistor_212 (.in(1'b0), .out(L_36_f906ff59), .gate(IR7));
  Transistor #(.\type ("n")) transistor_213 (.in(1'b0), .out(L_36_f906ff59), .gate(IR4));
  Pull_Resistor #(.pull(1)) pull_resistor_38 (.node(L_37_970560ea));
  Transistor #(.\type ("n")) transistor_214 (.in(1'b0), .out(L_37_970560ea), .gate(L_T4_1ff9fe8e));
  Transistor #(.\type ("n")) transistor_215 (.in(1'b0), .out(L_37_970560ea), .gate(or_1_out));
  Transistor #(.\type ("n")) transistor_216 (.in(1'b0), .out(L_37_970560ea), .gate(IR7));
  Transistor #(.\type ("n")) transistor_217 (.in(1'b0), .out(L_37_970560ea), .gate(IR4));
  Transistor #(.\type ("n")) transistor_218 (.in(1'b0), .out(L_37_970560ea), .gate(IR3));
  Transistor #(.\type ("n")) transistor_219 (.in(1'b0), .out(L_37_970560ea), .gate(IR2));
  Transistor #(.\type ("n")) transistor_220 (.in(1'b0), .out(L_37_970560ea), .gate(IR6));
  Pull_Resistor #(.pull(1)) pull_resistor_39 (.node(L_38_44e13d1d));
  Transistor #(.\type ("n")) transistor_221 (.in(1'b0), .out(L_38_44e13d1d), .gate(L_T4_1ff9fe8e));
  Transistor #(.\type ("n")) transistor_222 (.in(1'b0), .out(L_38_44e13d1d), .gate(or_1_out));
  Transistor #(.\type ("n")) transistor_223 (.in(1'b0), .out(L_38_44e13d1d), .gate(IR7));
  Transistor #(.\type ("n")) transistor_224 (.in(1'b0), .out(L_38_44e13d1d), .gate(IR4));
  Transistor #(.\type ("n")) transistor_225 (.in(1'b0), .out(L_38_44e13d1d), .gate(IR3));
  Transistor #(.\type ("n")) transistor_226 (.in(1'b0), .out(L_38_44e13d1d), .gate(IR2));
  Transistor #(.\type ("n")) transistor_227 (.in(1'b0), .out(L_38_44e13d1d), .gate(not_7_out));
  Transistor #(.\type ("n")) transistor_228 (.in(1'b0), .out(L_38_44e13d1d), .gate(IR5));
  Pull_Resistor #(.pull(1)) pull_resistor_40 (.node(L_39_ab49266d));
  Pull_Resistor #(.pull(1)) pull_resistor_41 (.node(L_40_b0ce7c4d));
  Transistor #(.\type ("n")) transistor_229 (.in(1'b0), .out(L_40_b0ce7c4d), .gate(L_T4_1ff9fe8e));
  Transistor #(.\type ("n")) transistor_230 (.in(1'b0), .out(L_39_ab49266d), .gate(L_T3_2730c10f));
  Transistor #(.\type ("n")) transistor_231 (.in(1'b0), .out(L_39_ab49266d), .gate(not_2_out));
  Transistor #(.\type ("n")) transistor_232 (.in(1'b0), .out(L_40_b0ce7c4d), .gate(not_2_out));
  Transistor #(.\type ("n")) transistor_233 (.in(1'b0), .out(L_39_ab49266d), .gate(IR4));
  Transistor #(.\type ("n")) transistor_234 (.in(1'b0), .out(L_40_b0ce7c4d), .gate(not_4_out));
  Transistor #(.\type ("n")) transistor_235 (.in(1'b0), .out(L_39_ab49266d), .gate(IR3));
  Transistor #(.\type ("n")) transistor_236 (.in(1'b0), .out(L_40_b0ce7c4d), .gate(IR3));
  Transistor #(.\type ("n")) transistor_237 (.in(1'b0), .out(L_39_ab49266d), .gate(IR2));
  Transistor #(.\type ("n")) transistor_238 (.in(1'b0), .out(L_40_b0ce7c4d), .gate(IR2));
  Pull_Resistor #(.pull(1)) pull_resistor_42 (.node(L_41_5ba99609));
  Transistor #(.\type ("n")) transistor_239 (.in(1'b0), .out(L_41_5ba99609), .gate(L_T2_2b20ddce));
  Transistor #(.\type ("n")) transistor_240 (.in(1'b0), .out(L_41_5ba99609), .gate(not_2_out));
  Transistor #(.\type ("n")) transistor_241 (.in(1'b0), .out(L_41_5ba99609), .gate(not_4_out));
  Transistor #(.\type ("n")) transistor_242 (.in(1'b0), .out(L_41_5ba99609), .gate(IR3));
  Transistor #(.\type ("n")) transistor_243 (.in(1'b0), .out(L_41_5ba99609), .gate(IR2));
  Pull_Resistor #(.pull(1)) pull_resistor_43 (.node(L_42_05de627d));
  Transistor #(.\type ("n")) transistor_244 (.in(1'b0), .out(L_42_05de627d), .gate(L_T3_2730c10f));
  Transistor #(.\type ("n")) transistor_245 (.in(1'b0), .out(L_42_05de627d), .gate(not_4_out));
  Transistor #(.\type ("n")) transistor_246 (.in(1'b0), .out(L_42_05de627d), .gate(not_5_out));
  Pull_Resistor #(.pull(1)) pull_resistor_44 (.node(L_43_e53210b4));
  Pull_Resistor #(.pull(1)) pull_resistor_45 (.node(L_44_7557d7f6));
  Transistor #(.\type ("n")) transistor_247 (.in(1'b0), .out(L_44_7557d7f6), .gate(not_1_out));
  Transistor #(.\type ("n")) transistor_248 (.in(1'b0), .out(L_43_e53210b4), .gate(or_1_out));
  Transistor #(.\type ("n")) transistor_249 (.in(1'b0), .out(L_43_e53210b4), .gate(IR7));
  Transistor #(.\type ("n")) transistor_250 (.in(1'b0), .out(L_44_7557d7f6), .gate(not_3_out));
  Transistor #(.\type ("n")) transistor_251 (.in(1'b0), .out(L_43_e53210b4), .gate(IR4));
  Transistor #(.\type ("n")) transistor_252 (.in(1'b0), .out(L_43_e53210b4), .gate(not_5_out));
  Transistor #(.\type ("n")) transistor_253 (.in(1'b0), .out(L_43_e53210b4), .gate(IR2));
  Transistor #(.\type ("n")) transistor_254 (.in(1'b0), .out(L_44_7557d7f6), .gate(not_7_out));
  Transistor #(.\type ("n")) transistor_255 (.in(1'b0), .out(L_43_e53210b4), .gate(not_8_out));
  Transistor #(.\type ("n")) transistor_256 (.in(1'b0), .out(L_44_7557d7f6), .gate(not_8_out));
  Pull_Resistor #(.pull(1)) pull_resistor_46 (.node(L_45_d477530d));
  Transistor #(.\type ("n")) transistor_257 (.in(1'b0), .out(L_45_d477530d), .gate(L_T4_1ff9fe8e));
  Transistor #(.\type ("n")) transistor_258 (.in(1'b0), .out(L_45_d477530d), .gate(not_2_out));
  Transistor #(.\type ("n")) transistor_259 (.in(1'b0), .out(L_45_d477530d), .gate(IR4));
  Transistor #(.\type ("n")) transistor_260 (.in(1'b0), .out(L_45_d477530d), .gate(IR3));
  Transistor #(.\type ("n")) transistor_261 (.in(1'b0), .out(L_45_d477530d), .gate(IR2));
  Pull_Resistor #(.pull(1)) pull_resistor_47 (.node(L_46_8026585c));
  Transistor #(.\type ("n")) transistor_262 (.in(1'b0), .out(L_46_8026585c), .gate(L_T3_2730c10f));
  Transistor #(.\type ("n")) transistor_263 (.in(1'b0), .out(L_46_8026585c), .gate(not_2_out));
  Transistor #(.\type ("n")) transistor_264 (.in(1'b0), .out(L_46_8026585c), .gate(not_4_out));
  Transistor #(.\type ("n")) transistor_265 (.in(1'b0), .out(L_46_8026585c), .gate(IR3));
  Transistor #(.\type ("n")) transistor_266 (.in(1'b0), .out(L_46_8026585c), .gate(IR2));
  Pull_Resistor #(.pull(1)) pull_resistor_48 (.node(L_47_50b9384c));
  Pull_Resistor #(.pull(1)) pull_resistor_49 (.node(L_48_961f2eda));
  Transistor #(.\type ("n")) transistor_267 (.in(1'b0), .out(L_48_961f2eda), .gate(L_T2_2b20ddce));
  Transistor #(.\type ("n")) transistor_268 (.in(1'b0), .out(L_47_50b9384c), .gate(or_1_out));
  Transistor #(.\type ("n")) transistor_269 (.in(1'b0), .out(L_48_961f2eda), .gate(or_1_out));
  Transistor #(.\type ("n")) transistor_270 (.in(1'b0), .out(L_47_50b9384c), .gate(IR7));
  Transistor #(.\type ("n")) transistor_271 (.in(1'b0), .out(L_48_961f2eda), .gate(IR7));
  Transistor #(.\type ("n")) transistor_272 (.in(1'b0), .out(L_47_50b9384c), .gate(IR4));
  Transistor #(.\type ("n")) transistor_273 (.in(1'b0), .out(L_48_961f2eda), .gate(IR4));
  Transistor #(.\type ("n")) transistor_274 (.in(1'b0), .out(L_47_50b9384c), .gate(IR3));
  Transistor #(.\type ("n")) transistor_275 (.in(1'b0), .out(L_48_961f2eda), .gate(IR3));
  Transistor #(.\type ("n")) transistor_276 (.in(1'b0), .out(L_47_50b9384c), .gate(IR2));
  Transistor #(.\type ("n")) transistor_277 (.in(1'b0), .out(L_48_961f2eda), .gate(IR2));
  Transistor #(.\type ("n")) transistor_278 (.in(1'b0), .out(L_48_961f2eda), .gate(IR6));
  Transistor #(.\type ("n")) transistor_279 (.in(1'b0), .out(L_47_50b9384c), .gate(not_7_out));
  Transistor #(.\type ("n")) transistor_280 (.in(1'b0), .out(L_48_961f2eda), .gate(not_8_out));
  Pull_Resistor #(.pull(1)) pull_resistor_50 (.node(L_49_b961b159));
  Transistor #(.\type ("n")) transistor_281 (.in(1'b0), .out(L_49_b961b159), .gate(or_1_out));
  Transistor #(.\type ("n")) transistor_282 (.in(1'b0), .out(L_49_b961b159), .gate(not_3_out));
  Transistor #(.\type ("n")) transistor_283 (.in(1'b0), .out(L_49_b961b159), .gate(IR4));
  Transistor #(.\type ("n")) transistor_284 (.in(1'b0), .out(L_49_b961b159), .gate(not_7_out));
  Transistor #(.\type ("n")) transistor_285 (.in(1'b0), .out(L_49_b961b159), .gate(L_T0_be2341f9));
  Pull_Resistor #(.pull(1)) pull_resistor_51 (.node(L_50_7cd0b929));
  Transistor #(.\type ("n")) transistor_286 (.in(1'b0), .out(L_50_7cd0b929), .gate(not_2_out));
  Transistor #(.\type ("n")) transistor_287 (.in(1'b0), .out(L_50_7cd0b929), .gate(not_3_out));
  Transistor #(.\type ("n")) transistor_288 (.in(1'b0), .out(L_50_7cd0b929), .gate(not_7_out));
  Transistor #(.\type ("n")) transistor_289 (.in(1'b0), .out(L_50_7cd0b929), .gate(IR5));
  Transistor #(.\type ("n")) transistor_290 (.in(1'b0), .out(L_50_7cd0b929), .gate(L_T0_be2341f9));
  Pull_Resistor #(.pull(1)) pull_resistor_52 (.node(L_51_73afc739));
  Pull_Resistor #(.pull(1)) pull_resistor_53 (.node(L_52_6bbb5c5f));
  Transistor #(.\type ("n")) transistor_291 (.in(1'b0), .out(L_51_73afc739), .gate(not_2_out));
  Transistor #(.\type ("n")) transistor_292 (.in(1'b0), .out(L_52_6bbb5c5f), .gate(not_2_out));
  Transistor #(.\type ("n")) transistor_293 (.in(1'b0), .out(L_51_73afc739), .gate(not_3_out));
  Transistor #(.\type ("n")) transistor_294 (.in(1'b0), .out(L_51_73afc739), .gate(not_7_out));
  Transistor #(.\type ("n")) transistor_295 (.in(1'b0), .out(L_52_6bbb5c5f), .gate(not_7_out));
  Transistor #(.\type ("n")) transistor_296 (.in(1'b0), .out(L_51_73afc739), .gate(not_8_out));
  Transistor #(.\type ("n")) transistor_297 (.in(1'b0), .out(L_52_6bbb5c5f), .gate(not_8_out));
  Transistor #(.\type ("n")) transistor_298 (.in(1'b0), .out(L_51_73afc739), .gate(L_T0_be2341f9));
  Transistor #(.\type ("n")) transistor_299 (.in(1'b0), .out(L_52_6bbb5c5f), .gate(L_T0_be2341f9));
  Pull_Resistor #(.pull(1)) pull_resistor_54 (.node(L_53_db17dfc3));
  Transistor #(.\type ("n")) transistor_300 (.in(1'b0), .out(L_53_db17dfc3), .gate(not_1_out));
  Transistor #(.\type ("n")) transistor_301 (.in(1'b0), .out(L_53_db17dfc3), .gate(IR7));
  Transistor #(.\type ("n")) transistor_302 (.in(1'b0), .out(L_53_db17dfc3), .gate(IR6));
  Transistor #(.\type ("n")) transistor_303 (.in(1'b0), .out(L_53_db17dfc3), .gate(not_8_out));
  Pull_Resistor #(.pull(1)) pull_resistor_55 (.node(L_54_df2d9682));
  Transistor #(.\type ("n")) transistor_304 (.in(1'b0), .out(L_54_df2d9682), .gate(L_T3_2730c10f));
  Transistor #(.\type ("n")) transistor_305 (.in(1'b0), .out(L_54_df2d9682), .gate(or_1_out));
  Transistor #(.\type ("n")) transistor_306 (.in(1'b0), .out(L_54_df2d9682), .gate(IR7));
  Transistor #(.\type ("n")) transistor_307 (.in(1'b0), .out(L_54_df2d9682), .gate(IR4));
  Transistor #(.\type ("n")) transistor_308 (.in(1'b0), .out(L_54_df2d9682), .gate(not_5_out));
  Transistor #(.\type ("n")) transistor_309 (.in(1'b0), .out(L_54_df2d9682), .gate(not_6_out));
  Transistor #(.\type ("n")) transistor_310 (.in(1'b0), .out(L_54_df2d9682), .gate(not_7_out));
  Pull_Resistor #(.pull(1)) pull_resistor_56 (.node(L_55_9656bee7));
  Pull_Resistor #(.pull(1)) pull_resistor_57 (.node(L_56_ff4a974b));
  Transistor #(.\type ("n")) transistor_311 (.in(1'b0), .out(L_56_ff4a974b), .gate(L_T5_e9d210fb));
  Transistor #(.\type ("n")) transistor_312 (.in(1'b0), .out(L_55_9656bee7), .gate(not_1_out));
  Transistor #(.\type ("n")) transistor_313 (.in(1'b0), .out(L_56_ff4a974b), .gate(or_1_out));
  Transistor #(.\type ("n")) transistor_314 (.in(1'b0), .out(L_55_9656bee7), .gate(IR7));
  Transistor #(.\type ("n")) transistor_315 (.in(1'b0), .out(L_56_ff4a974b), .gate(IR7));
  Transistor #(.\type ("n")) transistor_316 (.in(1'b0), .out(L_56_ff4a974b), .gate(IR4));
  Transistor #(.\type ("n")) transistor_317 (.in(1'b0), .out(L_56_ff4a974b), .gate(IR3));
  Transistor #(.\type ("n")) transistor_318 (.in(1'b0), .out(L_56_ff4a974b), .gate(IR2));
  Transistor #(.\type ("n")) transistor_319 (.in(1'b0), .out(L_55_9656bee7), .gate(IR6));
  Transistor #(.\type ("n")) transistor_320 (.in(1'b0), .out(L_56_ff4a974b), .gate(IR6));
  Transistor #(.\type ("n")) transistor_321 (.in(1'b0), .out(L_56_ff4a974b), .gate(not_8_out));
  Pull_Resistor #(.pull(1)) pull_resistor_58 (.node(L_57_bd139f3f));
  Transistor #(.\type ("n")) transistor_322 (.in(1'b0), .out(L_57_bd139f3f), .gate(L_T2_2b20ddce));
  Transistor #(.\type ("n")) transistor_323 (.in(1'b0), .out(L_57_bd139f3f), .gate(or_1_out));
  Transistor #(.\type ("n")) transistor_324 (.in(1'b0), .out(L_57_bd139f3f), .gate(IR7));
  Transistor #(.\type ("n")) transistor_325 (.in(1'b0), .out(L_57_bd139f3f), .gate(IR4));
  Transistor #(.\type ("n")) transistor_326 (.in(1'b0), .out(L_57_bd139f3f), .gate(IR2));
  Pull_Resistor #(.pull(1)) pull_resistor_59 (.node(L_58_b698ce08));
  Transistor #(.\type ("n")) transistor_327 (.in(1'b0), .out(L_58_b698ce08), .gate(or_1_out));
  Transistor #(.\type ("n")) transistor_328 (.in(1'b0), .out(L_58_b698ce08), .gate(not_3_out));
  Transistor #(.\type ("n")) transistor_329 (.in(1'b0), .out(L_58_b698ce08), .gate(not_4_out));
  Transistor #(.\type ("n")) transistor_330 (.in(1'b0), .out(L_58_b698ce08), .gate(not_5_out));
  Transistor #(.\type ("n")) transistor_331 (.in(1'b0), .out(L_58_b698ce08), .gate(IR2));
  Transistor #(.\type ("n")) transistor_332 (.in(1'b0), .out(L_58_b698ce08), .gate(IR6));
  Transistor #(.\type ("n")) transistor_333 (.in(1'b0), .out(L_58_b698ce08), .gate(IR5));
  Transistor #(.\type ("n")) transistor_334 (.in(1'b0), .out(L_58_b698ce08), .gate(L_T0_be2341f9));
  Pull_Resistor #(.pull(1)) pull_resistor_60 (.node(L_59_15390865));
  Pull_Resistor #(.pull(1)) pull_resistor_61 (.node(L_60_ba37dadc));
  Transistor #(.\type ("n")) transistor_335 (.in(1'b0), .out(L_59_15390865), .gate(not_2_out));
  Transistor #(.\type ("n")) transistor_336 (.in(1'b0), .out(L_60_ba37dadc), .gate(not_2_out));
  Transistor #(.\type ("n")) transistor_337 (.in(1'b0), .out(L_59_15390865), .gate(IR7));
  Transistor #(.\type ("n")) transistor_338 (.in(1'b0), .out(L_60_ba37dadc), .gate(not_7_out));
  Transistor #(.\type ("n")) transistor_339 (.in(1'b0), .out(L_60_ba37dadc), .gate(not_8_out));
  Transistor #(.\type ("n")) transistor_340 (.in(1'b0), .out(L_59_15390865), .gate(L_T1X_cd47d06e));
  Transistor #(.\type ("n")) transistor_341 (.in(1'b0), .out(L_60_ba37dadc), .gate(L_T1X_cd47d06e));
  Pull_Resistor #(.pull(1)) pull_resistor_62 (.node(L_61_aa3c3e0c));
  Transistor #(.\type ("n")) transistor_342 (.in(1'b0), .out(L_61_aa3c3e0c), .gate(not_1_out));
  Transistor #(.\type ("n")) transistor_343 (.in(1'b0), .out(L_61_aa3c3e0c), .gate(IR7));
  Transistor #(.\type ("n")) transistor_344 (.in(1'b0), .out(L_61_aa3c3e0c), .gate(IR4));
  Transistor #(.\type ("n")) transistor_345 (.in(1'b0), .out(L_61_aa3c3e0c), .gate(IR2));
  Transistor #(.\type ("n")) transistor_346 (.in(1'b0), .out(L_61_aa3c3e0c), .gate(L_T1X_cd47d06e));
  Pull_Resistor #(.pull(1)) pull_resistor_63 (.node(L_62_1cf1b605));
  Transistor #(.\type ("n")) transistor_347 (.in(1'b0), .out(L_62_1cf1b605), .gate(not_1_out));
  Transistor #(.\type ("n")) transistor_348 (.in(1'b0), .out(L_62_1cf1b605), .gate(not_3_out));
  Transistor #(.\type ("n")) transistor_349 (.in(1'b0), .out(L_62_1cf1b605), .gate(IR4));
  Transistor #(.\type ("n")) transistor_350 (.in(1'b0), .out(L_62_1cf1b605), .gate(not_5_out));
  Transistor #(.\type ("n")) transistor_351 (.in(1'b0), .out(L_62_1cf1b605), .gate(IR2));
  Transistor #(.\type ("n")) transistor_352 (.in(1'b0), .out(L_62_1cf1b605), .gate(IR6));
  Transistor #(.\type ("n")) transistor_353 (.in(1'b0), .out(L_62_1cf1b605), .gate(IR5));
  Transistor #(.\type ("n")) transistor_354 (.in(1'b0), .out(L_62_1cf1b605), .gate(L_T0_be2341f9));
  Pull_Resistor #(.pull(1)) pull_resistor_64 (.node(L_63_0219edaa));
  Pull_Resistor #(.pull(1)) pull_resistor_65 (.node(L_64_c9babf32));
  Transistor #(.\type ("n")) transistor_355 (.in(1'b0), .out(L_63_0219edaa), .gate(or_1_out));
  Transistor #(.\type ("n")) transistor_356 (.in(1'b0), .out(L_64_c9babf32), .gate(not_2_out));
  Transistor #(.\type ("n")) transistor_357 (.in(1'b0), .out(L_63_0219edaa), .gate(IR7));
  Transistor #(.\type ("n")) transistor_358 (.in(1'b0), .out(L_64_c9babf32), .gate(not_3_out));
  Transistor #(.\type ("n")) transistor_359 (.in(1'b0), .out(L_63_0219edaa), .gate(IR4));
  Transistor #(.\type ("n")) transistor_360 (.in(1'b0), .out(L_63_0219edaa), .gate(not_5_out));
  Transistor #(.\type ("n")) transistor_361 (.in(1'b0), .out(L_63_0219edaa), .gate(IR2));
  Transistor #(.\type ("n")) transistor_362 (.in(1'b0), .out(L_64_c9babf32), .gate(IR6));
  Transistor #(.\type ("n")) transistor_363 (.in(1'b0), .out(L_63_0219edaa), .gate(not_7_out));
  Transistor #(.\type ("n")) transistor_364 (.in(1'b0), .out(L_63_0219edaa), .gate(not_8_out));
  Transistor #(.\type ("n")) transistor_365 (.in(1'b0), .out(L_64_c9babf32), .gate(not_8_out));
  Transistor #(.\type ("n")) transistor_366 (.in(1'b0), .out(L_63_0219edaa), .gate(L_T0_be2341f9));
  Transistor #(.\type ("n")) transistor_367 (.in(1'b0), .out(L_64_c9babf32), .gate(L_T0_be2341f9));
  Pull_Resistor #(.pull(1)) pull_resistor_66 (.node(L_65_a97300ad));
  Transistor #(.\type ("n")) transistor_368 (.in(1'b0), .out(L_65_a97300ad), .gate(not_2_out));
  Transistor #(.\type ("n")) transistor_369 (.in(1'b0), .out(L_65_a97300ad), .gate(L_T0_be2341f9));
  Pull_Resistor #(.pull(1)) pull_resistor_67 (.node(L_66_53023e8d));
  Transistor #(.\type ("n")) transistor_370 (.in(1'b0), .out(L_66_53023e8d), .gate(or_1_out));
  Transistor #(.\type ("n")) transistor_371 (.in(1'b0), .out(L_66_53023e8d), .gate(not_3_out));
  Transistor #(.\type ("n")) transistor_372 (.in(1'b0), .out(L_66_53023e8d), .gate(IR4));
  Transistor #(.\type ("n")) transistor_373 (.in(1'b0), .out(L_66_53023e8d), .gate(not_5_out));
  Transistor #(.\type ("n")) transistor_374 (.in(1'b0), .out(L_66_53023e8d), .gate(IR2));
  Transistor #(.\type ("n")) transistor_375 (.in(1'b0), .out(L_66_53023e8d), .gate(IR6));
  Transistor #(.\type ("n")) transistor_376 (.in(1'b0), .out(L_66_53023e8d), .gate(not_8_out));
  Transistor #(.\type ("n")) transistor_377 (.in(1'b0), .out(L_66_53023e8d), .gate(L_T0_be2341f9));
  Pull_Resistor #(.pull(1)) pull_resistor_68 (.node(L_67_07e7e8b6));
  Pull_Resistor #(.pull(1)) pull_resistor_69 (.node(L_68_a93b1446));
  Transistor #(.\type ("n")) transistor_378 (.in(1'b0), .out(L_67_07e7e8b6), .gate(not_1_out));
  Transistor #(.\type ("n")) transistor_379 (.in(1'b0), .out(L_68_a93b1446), .gate(not_1_out));
  Transistor #(.\type ("n")) transistor_380 (.in(1'b0), .out(L_67_07e7e8b6), .gate(IR7));
  Transistor #(.\type ("n")) transistor_381 (.in(1'b0), .out(L_68_a93b1446), .gate(not_3_out));
  Transistor #(.\type ("n")) transistor_382 (.in(1'b0), .out(L_67_07e7e8b6), .gate(IR4));
  Transistor #(.\type ("n")) transistor_383 (.in(1'b0), .out(L_68_a93b1446), .gate(IR4));
  Transistor #(.\type ("n")) transistor_384 (.in(1'b0), .out(L_67_07e7e8b6), .gate(not_5_out));
  Transistor #(.\type ("n")) transistor_385 (.in(1'b0), .out(L_68_a93b1446), .gate(not_5_out));
  Transistor #(.\type ("n")) transistor_386 (.in(1'b0), .out(L_67_07e7e8b6), .gate(IR2));
  Transistor #(.\type ("n")) transistor_387 (.in(1'b0), .out(L_68_a93b1446), .gate(IR2));
  Transistor #(.\type ("n")) transistor_388 (.in(1'b0), .out(L_68_a93b1446), .gate(IR6));
  Transistor #(.\type ("n")) transistor_389 (.in(1'b0), .out(L_68_a93b1446), .gate(not_8_out));
  Transistor #(.\type ("n")) transistor_390 (.in(1'b0), .out(L_67_07e7e8b6), .gate(L_T0_be2341f9));
  Transistor #(.\type ("n")) transistor_391 (.in(1'b0), .out(L_68_a93b1446), .gate(L_T0_be2341f9));
  Pull_Resistor #(.pull(1)) pull_resistor_70 (.node(L_69_c6a8c7bd));
  Transistor #(.\type ("n")) transistor_392 (.in(1'b0), .out(L_69_c6a8c7bd), .gate(or_1_out));
  Transistor #(.\type ("n")) transistor_393 (.in(1'b0), .out(L_69_c6a8c7bd), .gate(IR7));
  Transistor #(.\type ("n")) transistor_394 (.in(1'b0), .out(L_69_c6a8c7bd), .gate(IR4));
  Transistor #(.\type ("n")) transistor_395 (.in(1'b0), .out(L_69_c6a8c7bd), .gate(not_6_out));
  Transistor #(.\type ("n")) transistor_396 (.in(1'b0), .out(L_69_c6a8c7bd), .gate(IR6));
  Transistor #(.\type ("n")) transistor_397 (.in(1'b0), .out(L_69_c6a8c7bd), .gate(not_8_out));
  Transistor #(.\type ("n")) transistor_398 (.in(1'b0), .out(L_69_c6a8c7bd), .gate(L_T0_be2341f9));
  Pull_Resistor #(.pull(1)) pull_resistor_71 (.node(L_70_14a93969));
  Transistor #(.\type ("n")) transistor_399 (.in(1'b0), .out(L_70_14a93969), .gate(not_2_out));
  Transistor #(.\type ("n")) transistor_400 (.in(1'b0), .out(L_70_14a93969), .gate(IR7));
  Transistor #(.\type ("n")) transistor_401 (.in(1'b0), .out(L_70_14a93969), .gate(IR6));
  Transistor #(.\type ("n")) transistor_402 (.in(1'b0), .out(L_70_14a93969), .gate(not_8_out));
  Transistor #(.\type ("n")) transistor_403 (.in(1'b0), .out(L_70_14a93969), .gate(L_T0_be2341f9));
  Pull_Resistor #(.pull(1)) pull_resistor_72 (.node(L_71_037940dd));
  Pull_Resistor #(.pull(1)) pull_resistor_73 (.node(L_72_65280ac2));
  Transistor #(.\type ("n")) transistor_404 (.in(1'b0), .out(L_72_65280ac2), .gate(L_T5_e9d210fb));
  Transistor #(.\type ("n")) transistor_405 (.in(1'b0), .out(L_71_037940dd), .gate(L_T4_1ff9fe8e));
  Transistor #(.\type ("n")) transistor_406 (.in(1'b0), .out(L_72_65280ac2), .gate(not_2_out));
  Transistor #(.\type ("n")) transistor_407 (.in(1'b0), .out(L_71_037940dd), .gate(not_4_out));
  Transistor #(.\type ("n")) transistor_408 (.in(1'b0), .out(L_72_65280ac2), .gate(not_4_out));
  Transistor #(.\type ("n")) transistor_409 (.in(1'b0), .out(L_72_65280ac2), .gate(IR3));
  Transistor #(.\type ("n")) transistor_410 (.in(1'b0), .out(L_71_037940dd), .gate(not_5_out));
  Transistor #(.\type ("n")) transistor_411 (.in(1'b0), .out(L_72_65280ac2), .gate(IR2));
  Pull_Resistor #(.pull(1)) pull_resistor_74 (.node(L_73_116545e2));
  Transistor #(.\type ("n")) transistor_412 (.in(1'b0), .out(L_73_116545e2), .gate(or_1_out));
  Transistor #(.\type ("n")) transistor_413 (.in(1'b0), .out(L_73_116545e2), .gate(not_4_out));
  Transistor #(.\type ("n")) transistor_414 (.in(1'b0), .out(L_73_116545e2), .gate(IR3));
  Transistor #(.\type ("n")) transistor_415 (.in(1'b0), .out(L_73_116545e2), .gate(IR2));
  Transistor #(.\type ("n")) transistor_416 (.in(1'b0), .out(L_73_116545e2), .gate(L_T0_be2341f9));
  Pull_Resistor #(.pull(1)) pull_resistor_75 (.node(L_74_8a887fe0));
  Pull_Resistor #(.pull(1)) pull_resistor_76 (.node(L_75_fbc631d3));
  Transistor #(.\type ("n")) transistor_417 (.in(1'b0), .out(L_74_8a887fe0), .gate(L_T2_2b20ddce));
  Transistor #(.\type ("n")) transistor_418 (.in(1'b0), .out(L_75_fbc631d3), .gate(not_1_out));
  Transistor #(.\type ("n")) transistor_419 (.in(1'b0), .out(L_74_8a887fe0), .gate(or_1_out));
  Transistor #(.\type ("n")) transistor_420 (.in(1'b0), .out(L_74_8a887fe0), .gate(IR7));
  Transistor #(.\type ("n")) transistor_421 (.in(1'b0), .out(L_75_fbc631d3), .gate(IR7));
  Transistor #(.\type ("n")) transistor_422 (.in(1'b0), .out(L_74_8a887fe0), .gate(IR4));
  Transistor #(.\type ("n")) transistor_423 (.in(1'b0), .out(L_75_fbc631d3), .gate(IR4));
  Transistor #(.\type ("n")) transistor_424 (.in(1'b0), .out(L_74_8a887fe0), .gate(not_5_out));
  Transistor #(.\type ("n")) transistor_425 (.in(1'b0), .out(L_75_fbc631d3), .gate(not_5_out));
  Transistor #(.\type ("n")) transistor_426 (.in(1'b0), .out(L_74_8a887fe0), .gate(IR2));
  Transistor #(.\type ("n")) transistor_427 (.in(1'b0), .out(L_75_fbc631d3), .gate(IR2));
  Transistor #(.\type ("n")) transistor_428 (.in(1'b0), .out(L_74_8a887fe0), .gate(not_7_out));
  Transistor #(.\type ("n")) transistor_429 (.in(1'b0), .out(L_75_fbc631d3), .gate(not_7_out));
  Transistor #(.\type ("n")) transistor_430 (.in(1'b0), .out(L_74_8a887fe0), .gate(IR5));
  Transistor #(.\type ("n")) transistor_431 (.in(1'b0), .out(L_75_fbc631d3), .gate(L_T0_be2341f9));
  Pull_Resistor #(.pull(1)) pull_resistor_77 (.node(L_76_0c9e8790));
  Transistor #(.\type ("n")) transistor_432 (.in(1'b0), .out(L_76_0c9e8790), .gate(not_1_out));
  Transistor #(.\type ("n")) transistor_433 (.in(1'b0), .out(L_76_0c9e8790), .gate(IR7));
  Transistor #(.\type ("n")) transistor_434 (.in(1'b0), .out(L_76_0c9e8790), .gate(not_7_out));
  Pull_Resistor #(.pull(1)) pull_resistor_78 (.node(L_77_8a8d3736));
  Transistor #(.\type ("n")) transistor_435 (.in(1'b0), .out(L_77_8a8d3736), .gate(L_T2_2b20ddce));
  Transistor #(.\type ("n")) transistor_436 (.in(1'b0), .out(L_77_8a8d3736), .gate(or_1_out));
  Transistor #(.\type ("n")) transistor_437 (.in(1'b0), .out(L_77_8a8d3736), .gate(IR7));
  Transistor #(.\type ("n")) transistor_438 (.in(1'b0), .out(L_77_8a8d3736), .gate(IR4));
  Transistor #(.\type ("n")) transistor_439 (.in(1'b0), .out(L_77_8a8d3736), .gate(IR3));
  Transistor #(.\type ("n")) transistor_440 (.in(1'b0), .out(L_77_8a8d3736), .gate(IR2));
  Transistor #(.\type ("n")) transistor_441 (.in(1'b0), .out(L_77_8a8d3736), .gate(IR6));
  Transistor #(.\type ("n")) transistor_442 (.in(1'b0), .out(L_77_8a8d3736), .gate(IR5));
  Pull_Resistor #(.pull(1)) pull_resistor_79 (.node(L_78_142fff2c));
  Pull_Resistor #(.pull(1)) pull_resistor_80 (.node(L_79_88caeb61));
  Transistor #(.\type ("n")) transistor_443 (.in(1'b0), .out(L_78_142fff2c), .gate(L_T3_2730c10f));
  Transistor #(.\type ("n")) transistor_444 (.in(1'b0), .out(L_78_142fff2c), .gate(or_1_out));
  Transistor #(.\type ("n")) transistor_445 (.in(1'b0), .out(L_79_88caeb61), .gate(not_2_out));
  Transistor #(.\type ("n")) transistor_446 (.in(1'b0), .out(L_78_142fff2c), .gate(IR7));
  Transistor #(.\type ("n")) transistor_447 (.in(1'b0), .out(L_79_88caeb61), .gate(not_3_out));
  Transistor #(.\type ("n")) transistor_448 (.in(1'b0), .out(L_78_142fff2c), .gate(IR4));
  Transistor #(.\type ("n")) transistor_449 (.in(1'b0), .out(L_78_142fff2c), .gate(IR3));
  Transistor #(.\type ("n")) transistor_450 (.in(1'b0), .out(L_78_142fff2c), .gate(IR2));
  Transistor #(.\type ("n")) transistor_451 (.in(1'b0), .out(L_78_142fff2c), .gate(IR6));
  Transistor #(.\type ("n")) transistor_452 (.in(1'b0), .out(L_79_88caeb61), .gate(IR6));
  Transistor #(.\type ("n")) transistor_453 (.in(1'b0), .out(L_79_88caeb61), .gate(IR5));
  Transistor #(.\type ("n")) transistor_454 (.in(1'b0), .out(L_78_142fff2c), .gate(not_8_out));
  Pull_Resistor #(.pull(1)) pull_resistor_81 (.node(L_80_442d40a3));
  Transistor #(.\type ("n")) transistor_455 (.in(1'b0), .out(L_80_442d40a3), .gate(L_T2_2b20ddce));
  Transistor #(.\type ("n")) transistor_456 (.in(1'b0), .out(L_80_442d40a3), .gate(or_1_out));
  Transistor #(.\type ("n")) transistor_457 (.in(1'b0), .out(L_80_442d40a3), .gate(not_4_out));
  Transistor #(.\type ("n")) transistor_458 (.in(1'b0), .out(L_80_442d40a3), .gate(IR3));
  Transistor #(.\type ("n")) transistor_459 (.in(1'b0), .out(L_80_442d40a3), .gate(IR2));
  Pull_Resistor #(.pull(1)) pull_resistor_82 (.node(L_81_7ac19b4f));
  Transistor #(.\type ("n")) transistor_460 (.in(1'b0), .out(L_81_7ac19b4f), .gate(L_T2_2b20ddce));
  Transistor #(.\type ("n")) transistor_461 (.in(1'b0), .out(L_81_7ac19b4f), .gate(IR3));
  Transistor #(.\type ("n")) transistor_462 (.in(1'b0), .out(L_81_7ac19b4f), .gate(not_6_out));
  Pull_Resistor #(.pull(1)) pull_resistor_83 (.node(L_82_53fd2612));
  Pull_Resistor #(.pull(1)) pull_resistor_84 (.node(L_83_8900340a));
  Transistor #(.\type ("n")) transistor_463 (.in(1'b0), .out(L_82_53fd2612), .gate(L_T2_2b20ddce));
  Transistor #(.\type ("n")) transistor_464 (.in(1'b0), .out(L_83_8900340a), .gate(L_T2_2b20ddce));
  Transistor #(.\type ("n")) transistor_465 (.in(1'b0), .out(L_82_53fd2612), .gate(not_2_out));
  Transistor #(.\type ("n")) transistor_466 (.in(1'b0), .out(L_82_53fd2612), .gate(IR3));
  Transistor #(.\type ("n")) transistor_467 (.in(1'b0), .out(L_83_8900340a), .gate(not_5_out));
  Transistor #(.\type ("n")) transistor_468 (.in(1'b0), .out(L_82_53fd2612), .gate(IR2));
  Pull_Resistor #(.pull(1)) pull_resistor_85 (.node(L_84_4e42f7b7));
  Transistor #(.\type ("n")) transistor_469 (.in(1'b0), .out(L_84_4e42f7b7), .gate(L_T5_e9d210fb));
  Transistor #(.\type ("n")) transistor_470 (.in(1'b0), .out(L_84_4e42f7b7), .gate(or_1_out));
  Transistor #(.\type ("n")) transistor_471 (.in(1'b0), .out(L_84_4e42f7b7), .gate(IR7));
  Transistor #(.\type ("n")) transistor_472 (.in(1'b0), .out(L_84_4e42f7b7), .gate(IR4));
  Transistor #(.\type ("n")) transistor_473 (.in(1'b0), .out(L_84_4e42f7b7), .gate(IR3));
  Transistor #(.\type ("n")) transistor_474 (.in(1'b0), .out(L_84_4e42f7b7), .gate(IR2));
  Transistor #(.\type ("n")) transistor_475 (.in(1'b0), .out(L_84_4e42f7b7), .gate(not_7_out));
  Transistor #(.\type ("n")) transistor_476 (.in(1'b0), .out(L_84_4e42f7b7), .gate(not_8_out));
  Pull_Resistor #(.pull(1)) pull_resistor_86 (.node(L_85_90e036dc));
  Transistor #(.\type ("n")) transistor_477 (.in(1'b0), .out(L_85_90e036dc), .gate(L_T4_1ff9fe8e));
  Pull_Resistor #(.pull(1)) pull_resistor_87 (.node(L_86_fae89fad));
  Pull_Resistor #(.pull(1)) pull_resistor_88 (.node(L_87_be04a52b));
  Transistor #(.\type ("n")) transistor_478 (.in(1'b0), .out(L_86_fae89fad), .gate(L_T3_2730c10f));
  Transistor #(.\type ("n")) transistor_479 (.in(1'b0), .out(L_87_be04a52b), .gate(or_1_out));
  Transistor #(.\type ("n")) transistor_480 (.in(1'b0), .out(L_87_be04a52b), .gate(IR7));
  Transistor #(.\type ("n")) transistor_481 (.in(1'b0), .out(L_87_be04a52b), .gate(IR4));
  Transistor #(.\type ("n")) transistor_482 (.in(1'b0), .out(L_87_be04a52b), .gate(IR3));
  Transistor #(.\type ("n")) transistor_483 (.in(1'b0), .out(L_87_be04a52b), .gate(IR2));
  Transistor #(.\type ("n")) transistor_484 (.in(1'b0), .out(L_87_be04a52b), .gate(IR5));
  Transistor #(.\type ("n")) transistor_485 (.in(1'b0), .out(L_87_be04a52b), .gate(L_T0_be2341f9));
  Pull_Resistor #(.pull(1)) pull_resistor_89 (.node(L_88_ae4b2cef));
  Transistor #(.\type ("n")) transistor_486 (.in(1'b0), .out(L_88_ae4b2cef), .gate(or_1_out));
  Transistor #(.\type ("n")) transistor_487 (.in(1'b0), .out(L_88_ae4b2cef), .gate(IR7));
  Transistor #(.\type ("n")) transistor_488 (.in(1'b0), .out(L_88_ae4b2cef), .gate(IR4));
  Transistor #(.\type ("n")) transistor_489 (.in(1'b0), .out(L_88_ae4b2cef), .gate(not_5_out));
  Transistor #(.\type ("n")) transistor_490 (.in(1'b0), .out(L_88_ae4b2cef), .gate(not_6_out));
  Transistor #(.\type ("n")) transistor_491 (.in(1'b0), .out(L_88_ae4b2cef), .gate(not_7_out));
  Transistor #(.\type ("n")) transistor_492 (.in(1'b0), .out(L_88_ae4b2cef), .gate(L_T0_be2341f9));
  Pull_Resistor #(.pull(1)) pull_resistor_90 (.node(L_89_f62eed49));
  Transistor #(.\type ("n")) transistor_493 (.in(1'b0), .out(L_89_f62eed49), .gate(L_T5_e9d210fb));
  Transistor #(.\type ("n")) transistor_494 (.in(1'b0), .out(L_89_f62eed49), .gate(not_2_out));
  Transistor #(.\type ("n")) transistor_495 (.in(1'b0), .out(L_89_f62eed49), .gate(IR4));
  Transistor #(.\type ("n")) transistor_496 (.in(1'b0), .out(L_89_f62eed49), .gate(IR3));
  Transistor #(.\type ("n")) transistor_497 (.in(1'b0), .out(L_89_f62eed49), .gate(IR2));
  Pull_Resistor #(.pull(1)) pull_resistor_91 (.node(L_90_d21e06c7));
  Transistor #(.\type ("n")) transistor_498 (.in(1'b0), .out(L_90_d21e06c7), .gate(L_T3_2730c10f));
  Transistor #(.\type ("n")) transistor_499 (.in(1'b0), .out(L_90_d21e06c7), .gate(not_5_out));
  Pull_Resistor #(.pull(1)) pull_resistor_92 (.node(L_91_1b0c0c3e));
  Transistor #(.\type ("n")) transistor_500 (.in(1'b0), .out(L_91_1b0c0c3e), .gate(L_T4_1ff9fe8e));
  Transistor #(.\type ("n")) transistor_501 (.in(1'b0), .out(L_91_1b0c0c3e), .gate(not_2_out));
  Transistor #(.\type ("n")) transistor_502 (.in(1'b0), .out(L_91_1b0c0c3e), .gate(not_4_out));
  Transistor #(.\type ("n")) transistor_503 (.in(1'b0), .out(L_91_1b0c0c3e), .gate(IR3));
  Transistor #(.\type ("n")) transistor_504 (.in(1'b0), .out(L_91_1b0c0c3e), .gate(IR2));
  Pull_Resistor #(.pull(1)) pull_resistor_93 (.node(L_92_0642b8ec));
  Transistor #(.\type ("n")) transistor_505 (.in(1'b0), .out(L_92_0642b8ec), .gate(L_T3_2730c10f));
  Transistor #(.\type ("n")) transistor_506 (.in(1'b0), .out(L_92_0642b8ec), .gate(not_4_out));
  Transistor #(.\type ("n")) transistor_507 (.in(1'b0), .out(L_92_0642b8ec), .gate(not_5_out));
  Pull_Resistor #(.pull(1)) pull_resistor_94 (.node(L_93_66c1bc08));
  Pull_Resistor #(.pull(1)) pull_resistor_95 (.node(L_94_c36cbd45));
  Transistor #(.\type ("n")) transistor_508 (.in(1'b0), .out(L_93_66c1bc08), .gate(L_T3_2730c10f));
  Transistor #(.\type ("n")) transistor_509 (.in(1'b0), .out(L_93_66c1bc08), .gate(or_1_out));
  Transistor #(.\type ("n")) transistor_510 (.in(1'b0), .out(L_94_c36cbd45), .gate(or_1_out));
  Transistor #(.\type ("n")) transistor_511 (.in(1'b0), .out(L_94_c36cbd45), .gate(IR7));
  Transistor #(.\type ("n")) transistor_512 (.in(1'b0), .out(L_94_c36cbd45), .gate(IR4));
  Transistor #(.\type ("n")) transistor_513 (.in(1'b0), .out(L_93_66c1bc08), .gate(not_4_out));
  Transistor #(.\type ("n")) transistor_514 (.in(1'b0), .out(L_93_66c1bc08), .gate(IR3));
  Transistor #(.\type ("n")) transistor_515 (.in(1'b0), .out(L_94_c36cbd45), .gate(IR3));
  Transistor #(.\type ("n")) transistor_516 (.in(1'b0), .out(L_93_66c1bc08), .gate(IR2));
  Transistor #(.\type ("n")) transistor_517 (.in(1'b0), .out(L_94_c36cbd45), .gate(IR2));
  Transistor #(.\type ("n")) transistor_518 (.in(1'b0), .out(L_94_c36cbd45), .gate(IR5));
  Pull_Resistor #(.pull(1)) pull_resistor_96 (.node(L_95_8b08e919));
  Transistor #(.\type ("n")) transistor_519 (.in(1'b0), .out(L_95_8b08e919), .gate(or_1_out));
  Transistor #(.\type ("n")) transistor_520 (.in(1'b0), .out(L_95_8b08e919), .gate(IR7));
  Transistor #(.\type ("n")) transistor_521 (.in(1'b0), .out(L_95_8b08e919), .gate(IR4));
  Transistor #(.\type ("n")) transistor_522 (.in(1'b0), .out(L_95_8b08e919), .gate(IR3));
  Transistor #(.\type ("n")) transistor_523 (.in(1'b0), .out(L_95_8b08e919), .gate(IR2));
  Transistor #(.\type ("n")) transistor_524 (.in(1'b0), .out(L_95_8b08e919), .gate(IR6));
  Transistor #(.\type ("n")) transistor_525 (.in(1'b0), .out(L_95_8b08e919), .gate(not_8_out));
  Pull_Resistor #(.pull(1)) pull_resistor_97 (.node(L_96_4be017a7));
  Transistor #(.\type ("n")) transistor_526 (.in(1'b0), .out(L_96_4be017a7), .gate(or_1_out));
  Transistor #(.\type ("n")) transistor_527 (.in(1'b0), .out(L_96_4be017a7), .gate(IR7));
  Transistor #(.\type ("n")) transistor_528 (.in(1'b0), .out(L_96_4be017a7), .gate(IR4));
  Transistor #(.\type ("n")) transistor_529 (.in(1'b0), .out(L_96_4be017a7), .gate(not_5_out));
  Transistor #(.\type ("n")) transistor_530 (.in(1'b0), .out(L_96_4be017a7), .gate(not_6_out));
  Transistor #(.\type ("n")) transistor_531 (.in(1'b0), .out(L_96_4be017a7), .gate(not_7_out));
  Pull_Resistor #(.pull(1)) pull_resistor_98 (.node(L_97_91c265e2));
  Transistor #(.\type ("n")) transistor_532 (.in(1'b0), .out(L_97_91c265e2), .gate(not_3_out));
  Transistor #(.\type ("n")) transistor_533 (.in(1'b0), .out(L_97_91c265e2), .gate(IR6));
  Transistor #(.\type ("n")) transistor_534 (.in(1'b0), .out(L_97_91c265e2), .gate(IR5));
  Pull_Resistor #(.pull(1)) pull_resistor_99 (.node(L_98_1dfb9b6f));
  Transistor #(.\type ("n")) transistor_535 (.in(1'b0), .out(L_98_1dfb9b6f), .gate(L_T4_1ff9fe8e));
  Transistor #(.\type ("n")) transistor_536 (.in(1'b0), .out(L_98_1dfb9b6f), .gate(or_1_out));
  Transistor #(.\type ("n")) transistor_537 (.in(1'b0), .out(L_98_1dfb9b6f), .gate(IR7));
  Transistor #(.\type ("n")) transistor_538 (.in(1'b0), .out(L_98_1dfb9b6f), .gate(IR4));
  Transistor #(.\type ("n")) transistor_539 (.in(1'b0), .out(L_98_1dfb9b6f), .gate(IR3));
  Transistor #(.\type ("n")) transistor_540 (.in(1'b0), .out(L_98_1dfb9b6f), .gate(IR2));
  Transistor #(.\type ("n")) transistor_541 (.in(1'b0), .out(L_98_1dfb9b6f), .gate(IR6));
  Transistor #(.\type ("n")) transistor_542 (.in(1'b0), .out(L_98_1dfb9b6f), .gate(IR5));
  Pull_Resistor #(.pull(1)) pull_resistor_100 (.node(L_99_0cc83ca0));
  Pull_Resistor #(.pull(1)) pull_resistor_101 (.node(L_100_35836628));
  Transistor #(.\type ("n")) transistor_543 (.in(1'b0), .out(L_99_0cc83ca0), .gate(L_T2_2b20ddce));
  Transistor #(.\type ("n")) transistor_544 (.in(1'b0), .out(L_100_35836628), .gate(L_T2_2b20ddce));
  Transistor #(.\type ("n")) transistor_545 (.in(1'b0), .out(L_99_0cc83ca0), .gate(or_1_out));
  Transistor #(.\type ("n")) transistor_546 (.in(1'b0), .out(L_100_35836628), .gate(or_1_out));
  Transistor #(.\type ("n")) transistor_547 (.in(1'b0), .out(L_99_0cc83ca0), .gate(IR7));
  Transistor #(.\type ("n")) transistor_548 (.in(1'b0), .out(L_100_35836628), .gate(IR7));
  Transistor #(.\type ("n")) transistor_549 (.in(1'b0), .out(L_99_0cc83ca0), .gate(IR4));
  Transistor #(.\type ("n")) transistor_550 (.in(1'b0), .out(L_100_35836628), .gate(IR4));
  Transistor #(.\type ("n")) transistor_551 (.in(1'b0), .out(L_99_0cc83ca0), .gate(not_5_out));
  Transistor #(.\type ("n")) transistor_552 (.in(1'b0), .out(L_100_35836628), .gate(not_5_out));
  Transistor #(.\type ("n")) transistor_553 (.in(1'b0), .out(L_99_0cc83ca0), .gate(IR2));
  Transistor #(.\type ("n")) transistor_554 (.in(1'b0), .out(L_100_35836628), .gate(IR2));
  Transistor #(.\type ("n")) transistor_555 (.in(1'b0), .out(L_99_0cc83ca0), .gate(IR6));
  Transistor #(.\type ("n")) transistor_556 (.in(1'b0), .out(L_99_0cc83ca0), .gate(IR5));
  Transistor #(.\type ("n")) transistor_557 (.in(1'b0), .out(L_100_35836628), .gate(IR5));
  Pull_Resistor #(.pull(1)) pull_resistor_102 (.node(L_101_9d393967));
  Transistor #(.\type ("n")) transistor_558 (.in(1'b0), .out(L_101_9d393967), .gate(L_T4_1ff9fe8e));
  Transistor #(.\type ("n")) transistor_559 (.in(1'b0), .out(L_101_9d393967), .gate(or_1_out));
  Transistor #(.\type ("n")) transistor_560 (.in(1'b0), .out(L_101_9d393967), .gate(IR7));
  Transistor #(.\type ("n")) transistor_561 (.in(1'b0), .out(L_101_9d393967), .gate(IR4));
  Transistor #(.\type ("n")) transistor_562 (.in(1'b0), .out(L_101_9d393967), .gate(not_5_out));
  Transistor #(.\type ("n")) transistor_563 (.in(1'b0), .out(L_101_9d393967), .gate(not_6_out));
  Transistor #(.\type ("n")) transistor_564 (.in(1'b0), .out(L_101_9d393967), .gate(not_7_out));
  Pull_Resistor #(.pull(1)) pull_resistor_103 (.node(L_102_881ca15e));
  Transistor #(.\type ("n")) transistor_565 (.in(1'b0), .out(L_102_881ca15e), .gate(L_T5_e9d210fb));
  Transistor #(.\type ("n")) transistor_566 (.in(1'b0), .out(L_102_881ca15e), .gate(or_1_out));
  Transistor #(.\type ("n")) transistor_567 (.in(1'b0), .out(L_102_881ca15e), .gate(IR7));
  Transistor #(.\type ("n")) transistor_568 (.in(1'b0), .out(L_102_881ca15e), .gate(IR4));
  Transistor #(.\type ("n")) transistor_569 (.in(1'b0), .out(L_102_881ca15e), .gate(IR3));
  Transistor #(.\type ("n")) transistor_570 (.in(1'b0), .out(L_102_881ca15e), .gate(IR2));
  Transistor #(.\type ("n")) transistor_571 (.in(1'b0), .out(L_102_881ca15e), .gate(not_7_out));
  Pull_Resistor #(.pull(1)) pull_resistor_104 (.node(L_103_46ba03e4));
  Transistor #(.\type ("n")) transistor_572 (.in(1'b0), .out(L_103_46ba03e4), .gate(L_T5_e9d210fb));
  Transistor #(.\type ("n")) transistor_573 (.in(1'b0), .out(L_103_46ba03e4), .gate(or_1_out));
  Transistor #(.\type ("n")) transistor_574 (.in(1'b0), .out(L_103_46ba03e4), .gate(IR7));
  Transistor #(.\type ("n")) transistor_575 (.in(1'b0), .out(L_103_46ba03e4), .gate(IR4));
  Transistor #(.\type ("n")) transistor_576 (.in(1'b0), .out(L_103_46ba03e4), .gate(IR3));
  Transistor #(.\type ("n")) transistor_577 (.in(1'b0), .out(L_103_46ba03e4), .gate(IR2));
  Transistor #(.\type ("n")) transistor_578 (.in(1'b0), .out(L_103_46ba03e4), .gate(IR6));
  Transistor #(.\type ("n")) transistor_579 (.in(1'b0), .out(L_103_46ba03e4), .gate(not_8_out));
  Pull_Resistor #(.pull(1)) pull_resistor_105 (.node(L_104_2077d36b));
  Pull_Resistor #(.pull(1)) pull_resistor_106 (.node(L_105_a29cdf8d));
  Transistor #(.\type ("n")) transistor_580 (.in(1'b0), .out(L_105_a29cdf8d), .gate(L_T3_2730c10f));
  Transistor #(.\type ("n")) transistor_581 (.in(1'b0), .out(L_104_2077d36b), .gate(L_T2_2b20ddce));
  Transistor #(.\type ("n")) transistor_582 (.in(1'b0), .out(L_104_2077d36b), .gate(or_1_out));
  Transistor #(.\type ("n")) transistor_583 (.in(1'b0), .out(L_105_a29cdf8d), .gate(or_1_out));
  Transistor #(.\type ("n")) transistor_584 (.in(1'b0), .out(L_104_2077d36b), .gate(IR7));
  Transistor #(.\type ("n")) transistor_585 (.in(1'b0), .out(L_105_a29cdf8d), .gate(IR7));
  Transistor #(.\type ("n")) transistor_586 (.in(1'b0), .out(L_104_2077d36b), .gate(IR4));
  Transistor #(.\type ("n")) transistor_587 (.in(1'b0), .out(L_105_a29cdf8d), .gate(IR4));
  Transistor #(.\type ("n")) transistor_588 (.in(1'b0), .out(L_104_2077d36b), .gate(not_5_out));
  Transistor #(.\type ("n")) transistor_589 (.in(1'b0), .out(L_105_a29cdf8d), .gate(not_5_out));
  Transistor #(.\type ("n")) transistor_590 (.in(1'b0), .out(L_105_a29cdf8d), .gate(IR2));
  Transistor #(.\type ("n")) transistor_591 (.in(1'b0), .out(L_104_2077d36b), .gate(not_6_out));
  Transistor #(.\type ("n")) transistor_592 (.in(1'b0), .out(L_104_2077d36b), .gate(not_7_out));
  Transistor #(.\type ("n")) transistor_593 (.in(1'b0), .out(L_104_2077d36b), .gate(IR5));
  Transistor #(.\type ("n")) transistor_594 (.in(1'b0), .out(L_105_a29cdf8d), .gate(not_8_out));
  Pull_Resistor #(.pull(1)) pull_resistor_107 (.node(L_106_36001eab));
  Transistor #(.\type ("n")) transistor_595 (.in(1'b0), .out(L_106_36001eab), .gate(not_1_out));
  Transistor #(.\type ("n")) transistor_596 (.in(1'b0), .out(L_106_36001eab), .gate(not_7_out));
  Pull_Resistor #(.pull(1)) pull_resistor_108 (.node(L_107_68d37105));
  Transistor #(.\type ("n")) transistor_597 (.in(1'b0), .out(L_107_68d37105), .gate(not_1_out));
  Transistor #(.\type ("n")) transistor_598 (.in(1'b0), .out(L_107_68d37105), .gate(IR7));
  Transistor #(.\type ("n")) transistor_599 (.in(1'b0), .out(L_107_68d37105), .gate(IR6));
  Pull_Resistor #(.pull(1)) pull_resistor_109 (.node(L_108_a15fa495));
  Transistor #(.\type ("n")) transistor_600 (.in(1'b0), .out(L_108_a15fa495), .gate(or_1_out));
  Transistor #(.\type ("n")) transistor_601 (.in(1'b0), .out(L_108_a15fa495), .gate(IR7));
  Transistor #(.\type ("n")) transistor_602 (.in(1'b0), .out(L_108_a15fa495), .gate(not_4_out));
  Transistor #(.\type ("n")) transistor_603 (.in(1'b0), .out(L_108_a15fa495), .gate(IR2));
  Transistor #(.\type ("n")) transistor_604 (.in(1'b0), .out(L_108_a15fa495), .gate(not_7_out));
  Transistor #(.\type ("n")) transistor_605 (.in(1'b0), .out(L_108_a15fa495), .gate(L_T0_be2341f9));
  Pull_Resistor #(.pull(1)) pull_resistor_110 (.node(L_109_8b0ee0a1));
  Transistor #(.\type ("n")) transistor_606 (.in(1'b0), .out(L_109_8b0ee0a1), .gate(or_1_out));
  Transistor #(.\type ("n")) transistor_607 (.in(1'b0), .out(L_109_8b0ee0a1), .gate(IR7));
  Transistor #(.\type ("n")) transistor_608 (.in(1'b0), .out(L_109_8b0ee0a1), .gate(IR4));
  Transistor #(.\type ("n")) transistor_609 (.in(1'b0), .out(L_109_8b0ee0a1), .gate(not_6_out));
  Transistor #(.\type ("n")) transistor_610 (.in(1'b0), .out(L_109_8b0ee0a1), .gate(IR6));
  Transistor #(.\type ("n")) transistor_611 (.in(1'b0), .out(L_109_8b0ee0a1), .gate(not_8_out));
  Transistor #(.\type ("n")) transistor_612 (.in(1'b0), .out(L_109_8b0ee0a1), .gate(L_T1X_cd47d06e));
  Pull_Resistor #(.pull(1)) pull_resistor_111 (.node(L_110_e7c60ed0));
  Pull_Resistor #(.pull(1)) pull_resistor_112 (.node(L_111_1042ad89));
  Transistor #(.\type ("n")) transistor_613 (.in(1'b0), .out(L_111_1042ad89), .gate(L_T3_2730c10f));
  Transistor #(.\type ("n")) transistor_614 (.in(1'b0), .out(L_110_e7c60ed0), .gate(or_1_out));
  Transistor #(.\type ("n")) transistor_615 (.in(1'b0), .out(L_110_e7c60ed0), .gate(IR7));
  Transistor #(.\type ("n")) transistor_616 (.in(1'b0), .out(L_110_e7c60ed0), .gate(not_4_out));
  Transistor #(.\type ("n")) transistor_617 (.in(1'b0), .out(L_111_1042ad89), .gate(not_4_out));
  Transistor #(.\type ("n")) transistor_618 (.in(1'b0), .out(L_111_1042ad89), .gate(IR3));
  Transistor #(.\type ("n")) transistor_619 (.in(1'b0), .out(L_110_e7c60ed0), .gate(not_5_out));
  Transistor #(.\type ("n")) transistor_620 (.in(1'b0), .out(L_110_e7c60ed0), .gate(IR2));
  Transistor #(.\type ("n")) transistor_621 (.in(1'b0), .out(L_111_1042ad89), .gate(not_6_out));
  Transistor #(.\type ("n")) transistor_622 (.in(1'b0), .out(L_110_e7c60ed0), .gate(IR6));
  Transistor #(.\type ("n")) transistor_623 (.in(1'b0), .out(L_110_e7c60ed0), .gate(L_T0_be2341f9));
  Pull_Resistor #(.pull(1)) pull_resistor_113 (.node(L_112_063f5ab4));
  Transistor #(.\type ("n")) transistor_624 (.in(1'b0), .out(L_112_063f5ab4), .gate(not_2_out));
  Transistor #(.\type ("n")) transistor_625 (.in(1'b0), .out(L_112_063f5ab4), .gate(not_7_out));
  Transistor #(.\type ("n")) transistor_626 (.in(1'b0), .out(L_112_063f5ab4), .gate(not_8_out));
  Transistor #(.\type ("n")) transistor_627 (.in(1'b0), .out(L_112_063f5ab4), .gate(L_T1X_cd47d06e));
  Pull_Resistor #(.pull(1)) pull_resistor_114 (.node(L_113_69d8438b));
  Transistor #(.\type ("n")) transistor_628 (.in(1'b0), .out(L_113_69d8438b), .gate(or_1_out));
  Transistor #(.\type ("n")) transistor_629 (.in(1'b0), .out(L_113_69d8438b), .gate(IR7));
  Transistor #(.\type ("n")) transistor_630 (.in(1'b0), .out(L_113_69d8438b), .gate(IR4));
  Transistor #(.\type ("n")) transistor_631 (.in(1'b0), .out(L_113_69d8438b), .gate(not_6_out));
  Transistor #(.\type ("n")) transistor_632 (.in(1'b0), .out(L_113_69d8438b), .gate(IR6));
  Transistor #(.\type ("n")) transistor_633 (.in(1'b0), .out(L_113_69d8438b), .gate(not_8_out));
  Transistor #(.\type ("n")) transistor_634 (.in(1'b0), .out(L_113_69d8438b), .gate(L_T0_be2341f9));
  Pull_Resistor #(.pull(1)) pull_resistor_115 (.node(L_114_a7bf33c8));
  Pull_Resistor #(.pull(1)) pull_resistor_116 (.node(L_115_0ffd4dd7));
  Transistor #(.\type ("n")) transistor_635 (.in(1'b0), .out(L_115_0ffd4dd7), .gate(L_T4_1ff9fe8e));
  Transistor #(.\type ("n")) transistor_636 (.in(1'b0), .out(L_114_a7bf33c8), .gate(or_1_out));
  Transistor #(.\type ("n")) transistor_637 (.in(1'b0), .out(L_115_0ffd4dd7), .gate(or_1_out));
  Transistor #(.\type ("n")) transistor_638 (.in(1'b0), .out(L_114_a7bf33c8), .gate(IR7));
  Transistor #(.\type ("n")) transistor_639 (.in(1'b0), .out(L_115_0ffd4dd7), .gate(IR7));
  Transistor #(.\type ("n")) transistor_640 (.in(1'b0), .out(L_114_a7bf33c8), .gate(IR4));
  Transistor #(.\type ("n")) transistor_641 (.in(1'b0), .out(L_115_0ffd4dd7), .gate(IR4));
  Transistor #(.\type ("n")) transistor_642 (.in(1'b0), .out(L_115_0ffd4dd7), .gate(IR3));
  Transistor #(.\type ("n")) transistor_643 (.in(1'b0), .out(L_114_a7bf33c8), .gate(not_5_out));
  Transistor #(.\type ("n")) transistor_644 (.in(1'b0), .out(L_114_a7bf33c8), .gate(IR2));
  Transistor #(.\type ("n")) transistor_645 (.in(1'b0), .out(L_115_0ffd4dd7), .gate(IR2));
  Transistor #(.\type ("n")) transistor_646 (.in(1'b0), .out(L_114_a7bf33c8), .gate(IR6));
  Transistor #(.\type ("n")) transistor_647 (.in(1'b0), .out(L_115_0ffd4dd7), .gate(not_7_out));
  Transistor #(.\type ("n")) transistor_648 (.in(1'b0), .out(L_115_0ffd4dd7), .gate(IR5));
  Transistor #(.\type ("n")) transistor_649 (.in(1'b0), .out(L_114_a7bf33c8), .gate(not_8_out));
  Transistor #(.\type ("n")) transistor_650 (.in(1'b0), .out(L_114_a7bf33c8), .gate(L_T0_be2341f9));
  Pull_Resistor #(.pull(1)) pull_resistor_117 (.node(L_116_f87463c5));
  Transistor #(.\type ("n")) transistor_651 (.in(1'b0), .out(L_116_f87463c5), .gate(not_2_out));
  Transistor #(.\type ("n")) transistor_652 (.in(1'b0), .out(L_116_f87463c5), .gate(not_3_out));
  Transistor #(.\type ("n")) transistor_653 (.in(1'b0), .out(L_116_f87463c5), .gate(not_7_out));
  Transistor #(.\type ("n")) transistor_654 (.in(1'b0), .out(L_116_f87463c5), .gate(IR5));
  Transistor #(.\type ("n")) transistor_655 (.in(1'b0), .out(L_116_f87463c5), .gate(L_T1X_cd47d06e));
  Pull_Resistor #(.pull(1)) pull_resistor_118 (.node(L_117_54ea7dab));
  Transistor #(.\type ("n")) transistor_656 (.in(1'b0), .out(L_117_54ea7dab), .gate(or_1_out));
  Transistor #(.\type ("n")) transistor_657 (.in(1'b0), .out(L_117_54ea7dab), .gate(not_3_out));
  Transistor #(.\type ("n")) transistor_658 (.in(1'b0), .out(L_117_54ea7dab), .gate(IR4));
  Transistor #(.\type ("n")) transistor_659 (.in(1'b0), .out(L_117_54ea7dab), .gate(not_5_out));
  Transistor #(.\type ("n")) transistor_660 (.in(1'b0), .out(L_117_54ea7dab), .gate(not_6_out));
  Transistor #(.\type ("n")) transistor_661 (.in(1'b0), .out(L_117_54ea7dab), .gate(not_7_out));
  Transistor #(.\type ("n")) transistor_662 (.in(1'b0), .out(L_117_54ea7dab), .gate(L_T1X_cd47d06e));
  Pull_Resistor #(.pull(1)) pull_resistor_119 (.node(L_118_25ed7443));
  Pull_Resistor #(.pull(1)) pull_resistor_120 (.node(L_119_bc2ca239));
  Transistor #(.\type ("n")) transistor_663 (.in(1'b0), .out(L_118_25ed7443), .gate(not_1_out));
  Transistor #(.\type ("n")) transistor_664 (.in(1'b0), .out(L_119_bc2ca239), .gate(or_1_out));
  Transistor #(.\type ("n")) transistor_665 (.in(1'b0), .out(L_118_25ed7443), .gate(IR7));
  Transistor #(.\type ("n")) transistor_666 (.in(1'b0), .out(L_119_bc2ca239), .gate(not_3_out));
  Transistor #(.\type ("n")) transistor_667 (.in(1'b0), .out(L_118_25ed7443), .gate(IR4));
  Transistor #(.\type ("n")) transistor_668 (.in(1'b0), .out(L_119_bc2ca239), .gate(IR4));
  Transistor #(.\type ("n")) transistor_669 (.in(1'b0), .out(L_119_bc2ca239), .gate(IR3));
  Transistor #(.\type ("n")) transistor_670 (.in(1'b0), .out(L_118_25ed7443), .gate(not_5_out));
  Transistor #(.\type ("n")) transistor_671 (.in(1'b0), .out(L_118_25ed7443), .gate(IR2));
  Transistor #(.\type ("n")) transistor_672 (.in(1'b0), .out(L_118_25ed7443), .gate(IR6));
  Transistor #(.\type ("n")) transistor_673 (.in(1'b0), .out(L_119_bc2ca239), .gate(not_7_out));
  Transistor #(.\type ("n")) transistor_674 (.in(1'b0), .out(L_118_25ed7443), .gate(L_T1X_cd47d06e));
  Transistor #(.\type ("n")) transistor_675 (.in(1'b0), .out(L_119_bc2ca239), .gate(L_T1X_cd47d06e));
  Pull_Resistor #(.pull(1)) pull_resistor_121 (.node(L_120_bf62daef));
  Pull_Resistor #(.pull(1)) pull_resistor_122 (.node(L_121_348bd5c4));
  Transistor #(.\type ("n")) transistor_676 (.in(1'b0), .out(L_120_bf62daef), .gate(or_1_out));
  Transistor #(.\type ("n")) transistor_677 (.in(1'b0), .out(L_120_bf62daef), .gate(not_3_out));
  Transistor #(.\type ("n")) transistor_678 (.in(1'b0), .out(L_120_bf62daef), .gate(not_4_out));
  Transistor #(.\type ("n")) transistor_679 (.in(1'b0), .out(L_120_bf62daef), .gate(not_5_out));
  Transistor #(.\type ("n")) transistor_680 (.in(1'b0), .out(L_120_bf62daef), .gate(IR2));
  Transistor #(.\type ("n")) transistor_681 (.in(1'b0), .out(L_121_348bd5c4), .gate(IR6));
  Transistor #(.\type ("n")) transistor_682 (.in(1'b0), .out(L_120_bf62daef), .gate(not_7_out));
  Transistor #(.\type ("n")) transistor_683 (.in(1'b0), .out(L_120_bf62daef), .gate(L_T0_be2341f9));
  Pull_Resistor #(.pull(1)) pull_resistor_123 (.node(L_122_2b9e98b2));
  Transistor #(.\type ("n")) transistor_684 (.in(1'b0), .out(L_122_2b9e98b2), .gate(L_T3_2730c10f));
  Transistor #(.\type ("n")) transistor_685 (.in(1'b0), .out(L_122_2b9e98b2), .gate(IR4));
  Transistor #(.\type ("n")) transistor_686 (.in(1'b0), .out(L_122_2b9e98b2), .gate(not_5_out));
  Transistor #(.\type ("n")) transistor_687 (.in(1'b0), .out(L_122_2b9e98b2), .gate(not_6_out));
  Pull_Resistor #(.pull(1)) pull_resistor_124 (.node(L_123_ea048c49));
  Transistor #(.\type ("n")) transistor_688 (.in(1'b0), .out(L_123_ea048c49), .gate(L_T2_2b20ddce));
  Transistor #(.\type ("n")) transistor_689 (.in(1'b0), .out(L_123_ea048c49), .gate(IR4));
  Transistor #(.\type ("n")) transistor_690 (.in(1'b0), .out(L_123_ea048c49), .gate(IR3));
  Transistor #(.\type ("n")) transistor_691 (.in(1'b0), .out(L_123_ea048c49), .gate(not_6_out));
  Pull_Resistor #(.pull(1)) pull_resistor_125 (.node(L_124_3cfed9ae));
  Pull_Resistor #(.pull(1)) pull_resistor_126 (.node(L_125_0b8e34b8));
  Transistor #(.\type ("n")) transistor_692 (.in(1'b0), .out(L_124_3cfed9ae), .gate(L_T5_e9d210fb));
  Transistor #(.\type ("n")) transistor_693 (.in(1'b0), .out(L_125_0b8e34b8), .gate(L_T4_1ff9fe8e));
  Transistor #(.\type ("n")) transistor_694 (.in(1'b0), .out(L_124_3cfed9ae), .gate(not_2_out));
  Transistor #(.\type ("n")) transistor_695 (.in(1'b0), .out(L_125_0b8e34b8), .gate(not_4_out));
  Transistor #(.\type ("n")) transistor_696 (.in(1'b0), .out(L_124_3cfed9ae), .gate(IR3));
  Transistor #(.\type ("n")) transistor_697 (.in(1'b0), .out(L_125_0b8e34b8), .gate(not_5_out));
  Transistor #(.\type ("n")) transistor_698 (.in(1'b0), .out(L_124_3cfed9ae), .gate(IR2));
  Pull_Resistor #(.pull(1)) pull_resistor_127 (.node(L_126_b55b24f6));
  Transistor #(.\type ("n")) transistor_699 (.in(1'b0), .out(L_126_b55b24f6), .gate(IR7));
  Pull_Resistor #(.pull(1)) pull_resistor_128 (.node(L_127_f6767dc7));
  Transistor #(.\type ("n")) transistor_700 (.in(1'b0), .out(L_127_f6767dc7), .gate(or_1_out));
  Transistor #(.\type ("n")) transistor_701 (.in(1'b0), .out(L_127_f6767dc7), .gate(not_3_out));
  Transistor #(.\type ("n")) transistor_702 (.in(1'b0), .out(L_127_f6767dc7), .gate(not_4_out));
  Transistor #(.\type ("n")) transistor_703 (.in(1'b0), .out(L_127_f6767dc7), .gate(not_5_out));
  Transistor #(.\type ("n")) transistor_704 (.in(1'b0), .out(L_127_f6767dc7), .gate(IR2));
  Transistor #(.\type ("n")) transistor_705 (.in(1'b0), .out(L_127_f6767dc7), .gate(IR6));
  Transistor #(.\type ("n")) transistor_706 (.in(1'b0), .out(L_127_f6767dc7), .gate(not_8_out));
  Pull_Resistor #(.pull(1)) pull_resistor_129 (.node(L_128_aad3a25e));
  Pull_Resistor #(.pull(1)) pull_resistor_130 (.node(L_129_8838ebbd));
  Transistor #(.\type ("n")) transistor_707 (.in(1'b0), .out(L_128_aad3a25e), .gate(IR0));
  Transistor #(.\type ("n")) transistor_708 (.in(1'b0), .out(L_129_8838ebbd), .gate(or_1_out));
  Transistor #(.\type ("n")) transistor_709 (.in(1'b0), .out(L_129_8838ebbd), .gate(IR7));
  Transistor #(.\type ("n")) transistor_710 (.in(1'b0), .out(L_129_8838ebbd), .gate(IR4));
  Transistor #(.\type ("n")) transistor_711 (.in(1'b0), .out(L_128_aad3a25e), .gate(not_5_out));
  Transistor #(.\type ("n")) transistor_712 (.in(1'b0), .out(L_129_8838ebbd), .gate(not_5_out));
  Transistor #(.\type ("n")) transistor_713 (.in(1'b0), .out(L_128_aad3a25e), .gate(IR2));
  Transistor #(.\type ("n")) transistor_714 (.in(1'b0), .out(L_129_8838ebbd), .gate(IR2));

  // Notes on the sheet:
  //   TODO: Move IR0 to random logic
endmodule

module PREDECODE (
  input  PHI2,
  input  L_0_IR_fde7bd13,
  input  D0,
  input  D1,
  input  D2,
  input  D3,
  input  D4,
  input  D5,
  input  D6,
  input  D7,
  output L_IMPLIED_7f832bff,
  output L_TWOCYCLE_43089fae,
  output L_PD0_72855f64,
  output L_PD1_c99f14c8,
  output L_PD2_8bc41618,
  output L_PD3_ba6a24ea,
  output L_PD4_9583460c,
  output L_PD5_8dc63d2b,
  output L_PD6_87750ded,
  output L_PD7_40cf097f
);

  wire d_latch_6baf82dd_1_q, d_latch_6baf82dd_2_q, d_latch_6baf82dd_3_q, d_latch_6baf82dd_4_q,
       d_latch_6baf82dd_5_q, d_latch_6baf82dd_6_q, d_latch_6baf82dd_7_q, d_latch_6baf82dd_8_q, nand1_out,
       nor1_out, nor2_out, nor3_out, nor4_out, nor5_out, nor_1_out, nor_2_out, nor_3_out, nor_4_out,
       nor_5_out, nor_6_out, nor_7_out, nor_8_out, not_1_out, not_2_out, not_3_out, not_4_out, not_5_out,
       not_6_out, not_7_out, not_8_out, not_9_out, not_10_out, not_11_out, not_12_out, not_21_out;

  not not_1 (not_1_out, D0);
  not not_2 (not_2_out, D1);
  not not_3 (not_3_out, D2);
  not not_4 (not_4_out, D3);
  not not_5 (not_5_out, D4);
  not not_6 (not_6_out, D5);
  not not_7 (not_7_out, D6);
  not not_8 (not_8_out, D7);
  D_latch_6baf82dd d_latch_6baf82dd_1 (.Q(d_latch_6baf82dd_1_q), .D(not_1_out), .EN(PHI2));  // open: NOT_Q
  D_latch_6baf82dd d_latch_6baf82dd_2 (.Q(d_latch_6baf82dd_2_q), .D(not_2_out), .EN(PHI2));  // open: NOT_Q
  D_latch_6baf82dd d_latch_6baf82dd_3 (.Q(d_latch_6baf82dd_3_q), .D(not_3_out), .EN(PHI2));  // open: NOT_Q
  D_latch_6baf82dd d_latch_6baf82dd_4 (.Q(d_latch_6baf82dd_4_q), .D(not_4_out), .EN(PHI2));  // open: NOT_Q
  D_latch_6baf82dd d_latch_6baf82dd_5 (.Q(d_latch_6baf82dd_5_q), .D(not_5_out), .EN(PHI2));  // open: NOT_Q
  D_latch_6baf82dd d_latch_6baf82dd_6 (.Q(d_latch_6baf82dd_6_q), .D(not_6_out), .EN(PHI2));  // open: NOT_Q
  D_latch_6baf82dd d_latch_6baf82dd_7 (.Q(d_latch_6baf82dd_7_q), .D(not_7_out), .EN(PHI2));  // open: NOT_Q
  D_latch_6baf82dd d_latch_6baf82dd_8 (.Q(d_latch_6baf82dd_8_q), .D(not_8_out), .EN(PHI2));  // open: NOT_Q
  nor nor_1 (nor_1_out, d_latch_6baf82dd_1_q, L_0_IR_fde7bd13);
  nor nor_2 (nor_2_out, d_latch_6baf82dd_2_q, L_0_IR_fde7bd13);
  nor nor_3 (nor_3_out, d_latch_6baf82dd_3_q, L_0_IR_fde7bd13);
  nor nor_4 (nor_4_out, d_latch_6baf82dd_4_q, L_0_IR_fde7bd13);
  nor nor_5 (nor_5_out, d_latch_6baf82dd_5_q, L_0_IR_fde7bd13);
  nor nor_6 (nor_6_out, d_latch_6baf82dd_6_q, L_0_IR_fde7bd13);
  nor nor_7 (nor_7_out, d_latch_6baf82dd_7_q, L_0_IR_fde7bd13);
  nor nor_8 (nor_8_out, d_latch_6baf82dd_8_q, L_0_IR_fde7bd13);
  nor nor1 (nor1_out, nor_1_out, nor_3_out, not_9_out);
  not not_9 (not_9_out, nor_4_out);
  not not_10 (not_10_out, nor_1_out);
  nor nor2 (nor2_out, nor_2_out, nor_5_out, nor_8_out);
  nor nor3 (nor3_out, not_10_out, nor_3_out, not_11_out, nor_5_out);
  not not_11 (not_11_out, nor_4_out);
  nor nor4 (nor4_out, nor_1_out, not_12_out);
  not not_12 (not_12_out, nor_8_out);
  not not_13 (L_PD0_72855f64, nor_1_out);
  not not_14 (L_PD1_c99f14c8, nor_2_out);
  not not_15 (L_PD2_8bc41618, nor_3_out);
  not not_16 (L_PD3_ba6a24ea, nor_4_out);
  not not_17 (L_PD4_9583460c, nor_5_out);
  not not_18 (L_PD5_8dc63d2b, nor_6_out);
  not not_19 (L_PD6_87750ded, nor_7_out);
  not not_20 (L_PD7_40cf097f, nor_8_out);
  not not_21 (not_21_out, nor2_out);
  nand nand1 (nand1_out, nor1_out, not_21_out);
  nor nor5 (nor5_out, nor3_out, nor4_out);
  not not_22 (L_IMPLIED_7f832bff, nor1_out);
  and and9 (L_TWOCYCLE_43089fae, nand1_out, nor5_out);
endmodule

module RANDOM_LOGIC (
  input  PHI1,
  input  X0,
  input  X1,
  input  X2,
  input  X3,
  input  X4,
  input  X5,
  input  X6,
  input  X7,
  input  X8,
  input  X9,
  input  X10,
  input  X11,
  input  X12,
  input  X13,
  input  X14,
  input  X15,
  input  X16,
  input  X17,
  input  X18,
  input  X19,
  input  X20,
  input  X21,
  input  X22,
  input  X23,
  input  X24,
  input  X25,
  input  X26,
  input  X27,
  input  X28,
  input  X29,
  input  X30,
  input  X31,
  input  X32,
  input  X33,
  input  X34,
  input  X35,
  input  X36,
  input  X37,
  input  X38,
  input  X39,
  input  X40,
  input  X41,
  input  X42,
  input  X43,
  input  X44,
  input  X45,
  input  X46,
  input  X47,
  input  X48,
  input  X49,
  input  X50,
  input  X51,
  input  X52,
  input  X53,
  input  X54,
  input  X55,
  input  X56,
  input  X57,
  input  X58,
  input  X59,
  input  X60,
  input  X61,
  input  X62,
  input  X63,
  input  X64,
  input  X65,
  input  X66,
  input  X67,
  input  X68,
  input  X69,
  input  X70,
  input  X71,
  input  X72,
  input  X73,
  input  X74,
  input  X75,
  input  X76,
  input  X77,
  input  X78,
  input  X79,
  input  X80,
  input  X81,
  input  X82,
  input  X83,
  input  X84,
  input  X85,
  input  X86,
  input  X87,
  input  X88,
  input  X89,
  input  X90,
  input  X91,
  input  X92,
  input  X93,
  input  X94,
  input  X95,
  input  X96,
  input  X97,
  input  X98,
  input  X99,
  input  X100,
  input  X101,
  input  X102,
  input  X103,
  input  X104,
  input  X105,
  input  X106,
  input  X107,
  input  X108,
  input  X109,
  input  X110,
  input  X111,
  input  X112,
  input  X113,
  input  X114,
  input  X115,
  input  X116,
  input  X117,
  input  X118,
  input  X119,
  input  X120,
  input  X121,
  input  X122,
  input  X123,
  input  X124,
  input  X125,
  input  X126,
  input  X127,
  input  X128,
  input  X129,
  input  PHI2,
  input  L_IR5_7bf6fd52,
  input  L_NMIP_e9ae5a44,
  input  RESP,
  input  L_IRQP_906cd47b,
  input  AVR,
  input  ACR,
  input  SO,
  input  L_TWOCYCLE_43089fae,
  input  L_IMPLIED_7f832bff,
  input  RDY,
  input  L_PRDY_7910aae2,
  input  DB7,
  input  in_145,
  input  DB5,
  input  DB4,
  input  in_148,
  input  in_149,
  input  in_150,
  input  in_151,
  output FETCH,
  output L_T0_be2341f9,
  output L_T2_2b20ddce,
  output L_T3_2730c10f,
  output L_T4_1ff9fe8e,
  output L_T5_e9d210fb,
  output L_0_ADL0_372ea1ce,
  output L_0_ADL1_1828b789,
  output L_0_ADL2_a1d2ebaa,
  output Y_SB_981fc62c,
  output X_SB_50e8fb84,
  output SB_Y_f952d371,
  output SB_X_a4a389b1,
  output S_SB_c8f0deaa,
  output S_ADL_299349f9,
  output SB_S_e7e7b943,
  output S_S_0e77937e,
  output L_V_OUT_cf6c2405,
  output L_I_OUT_a88ea15a,
  output L_D_OUT_eaa1b777,
  output L_C_OUT_e01a0d59,
  output L_N_OUT_f0a30453,
  output L_Z_OUT_273329d7,
  output NDB_ADD_5826378a,
  output DB_ADD_49072aec,
  output L_0_ADD_7d0d5e3b,
  output SB_ADD_21cc08e7,
  output ADL_ADD_b3e2e6b8,
  output ANDS,
  output EORS,
  output ORS,
  output L_ACIN_e8912140,
  output SUMS,
  output L_DAA_9902be4a,
  output ADD_SB7_3b72c6f5,
  output ADD_SB06_79b3146b,
  output ADD_ADL_d25cdcd8,
  output L_DSA_8e87f2a8,
  output SRS,
  output DL_ADL_73e48c13,
  output DL_DB_4a6f16a8,
  output DL_ADH_067137e0,
  output ADH_ABH_4fac1902,
  output ADL_ABL_ccbf1bfb,
  output SB_AC_692b76aa,
  output AC_SB_4f3a8e20,
  output L_0_ADH0_8d3f04fb,
  output L_0_ADH17_42b6e0bd,
  output AC_DB_7461a43f,
  output SB_DB_92ea0e91,
  output SB_ADH_3fc727a4,
  output ADL_PCL_0d330abd,
  output PCL_PCL_effd7227,
  output PCH_ADH_329c7fb7,
  output PCL_ADL_75837bef,
  output PCH_DB_4d5eb992,
  output PCL_DB_8c5417e4,
  output ADH_PCH_413c8ef5,
  output PCH_PCH_e0d1ea0f,
  output TRESX,
  output L_0_IR_fde7bd13,
  output ENDS,
  output ENDX,
  output TRES1,
  output T1,
  output L_T1X_cd47d06e,
  output TRES2,
  output L_1_PC_f7ea2184,
  output P_DB_0ea80532,
  output IR5_I_a8b17eb4,
  output IR5_C_bb157132,
  output IR5_D_a37efeb0,
  output L_0_V_6d5b0af2,
  output ACR_C_fc5559e8,
  output DBZ_Z_805d2a94,
  output DB_N_4f1ad326,
  output DB_P_0fe10735,
  output DB_C_acfbba71,
  output DB_V_9eaeb3a2,
  output WR,
  output out_232,
  output DB6,
  output out_234,
  output out_235,
  output DB3,
  output DB2,
  output DB1,
  output DB0
);

  wire alu_setup_1_and, alu_setup_1_inc_sb, alu_setup_1_sr, BR0, branch_logic_1_brfw,
       branch_logic_1_l_brtaken_2a78ebe8, BRK6E, bus_control_1_pgx, bus_control_1_ztst, dispatch_1_acrl2,
       dispatch_1_stor, INTERRUPT_RESET_CONTROL_b_out, INTERRUPT_RESET_CONTROL_brk5_rdy,
       INTERRUPT_RESET_CONTROL_brk7, INTERRUPT_RESET_CONTROL_dores, INTERRUPT_RESET_CONTROL_l_donmi_539abb0d,
       L_READY_29998178, pc_setup_1_dl_pch_8d3d82e3, pc_setup_1_l_adl_pcl_8a671021,
       pc_setup_1_l_pch_pch_45eb8196, pc_setup_1_pc_db_528571a6, regs_control_1_sbxy, regs_control_1_stkop,
       regs_control_1_stxy, T0, T5, T6;

  INT_RESET_CONTROL INTERRUPT_RESET_CONTROL (
    .B_OUT(INTERRUPT_RESET_CONTROL_b_out), .BRK6E(BRK6E), .BRK7(INTERRUPT_RESET_CONTROL_brk7),
    .BRK5_RDY(INTERRUPT_RESET_CONTROL_brk5_rdy), .DORES(INTERRUPT_RESET_CONTROL_dores),
    .L_DONMI_539abb0d(INTERRUPT_RESET_CONTROL_l_donmi_539abb0d), .BR2(X80), .T0(T0),
    .L_IRQP_906cd47b(L_IRQP_906cd47b), .L_I_OUT_a88ea15a(L_I_OUT_a88ea15a), .BRK5(X22),
    .L_ready_2ba3d9e7(L_READY_29998178), .PHI1(PHI1), .RESP(RESP), .PHI2(PHI2),
    .L_NMIP_e9ae5a44(L_NMIP_e9ae5a44));
  INT_VECTOR INTERRUPT_VECTOR (
    .L_0_ADL0_372ea1ce(L_0_ADL0_372ea1ce), .L_0_ADL1_1828b789(L_0_ADL1_1828b789),
    .L_0_ADL2_a1d2ebaa(L_0_ADL2_a1d2ebaa), .PHI2(PHI2), .BRK5_RDY(INTERRUPT_RESET_CONTROL_brk5_rdy),
    .BRK7(INTERRUPT_RESET_CONTROL_brk7), .DORES(INTERRUPT_RESET_CONTROL_dores),
    .L_DONMI_539abb0d(INTERRUPT_RESET_CONTROL_l_donmi_539abb0d));
  REGS_CONTROL regs_control_1 (
    .S_ADL_299349f9(S_ADL_299349f9), .Y_SB_981fc62c(Y_SB_981fc62c), .STXY(regs_control_1_stxy),
    .X_SB_50e8fb84(X_SB_50e8fb84), .S_SB_c8f0deaa(S_SB_c8f0deaa), .SB_X_a4a389b1(SB_X_a4a389b1),
    .SBXY(regs_control_1_sbxy), .SB_Y_f952d371(SB_Y_f952d371), .SB_S_e7e7b943(SB_S_e7e7b943),
    .S_S_0e77937e(S_S_0e77937e), .STKOP(regs_control_1_stkop), .STOR(dispatch_1_stor), .D35(X35), .D0(X0),
    .D1(X1), .D2(X2), .D3(X3), .D4(X4), .D5(X5), .D6(X6), .D7(X7), .D8(X8), .PHI1(PHI1), .D9(X9), .D10(X10),
    .D11(X11), .D12(X12), .D13(X13), .D14(X14), .D15(X15), .D16(X16), .D17(X17), .D18(X18), .PHI2(PHI2),
    .D19(X19), .D20(X20), .D21(X21), .D22(X22), .D23(X23), .D24(X24), .D25(X25), .D26(X26), .D48(X48),
    .L_ready_2ba3d9e7(L_READY_29998178));
  FLAGS flags_1 (
    .DB0(DB0), .DB1(DB1), .DB2(DB2), .DB3(DB3), .out_33(out_235), .N_C(out_234), .DB6(DB6), .DB7(out_232),
    .L_Z_OUT_273329d7(L_Z_OUT_273329d7), .L_N_OUT_f0a30453(L_N_OUT_f0a30453),
    .L_C_OUT_e01a0d59(L_C_OUT_e01a0d59), .L_D_OUT_eaa1b777(L_D_OUT_eaa1b777),
    .L_I_OUT_a88ea15a(L_I_OUT_a88ea15a), .L_V_OUT_cf6c2405(L_V_OUT_cf6c2405),
    .L_IR5_7bf6fd52(L_IR5_7bf6fd52), .in_3(in_151), .IR5_I_a8b17eb4(IR5_I_a8b17eb4), .BRK6E(BRK6E),
    .AVR(AVR), .DB_V_9eaeb3a2(DB_V_9eaeb3a2), .D112(X112), .L_0_V_6d5b0af2(L_0_V_6d5b0af2), .in_4(in_150),
    .SO(SO), .in_5(in_149), .in_6(in_148), .DB4(DB4), .P_DB_0ea80532(P_DB_0ea80532), .DB5(DB5),
    .in_9(in_145), .in_10(DB7), .DB_P_0fe10735(DB_P_0fe10735), .DBZ_Z_805d2a94(DBZ_Z_805d2a94),
    .DB_N_4f1ad326(DB_N_4f1ad326), .IR5_C_bb157132(IR5_C_bb157132), .ACR(ACR),
    .B_OUT(INTERRUPT_RESET_CONTROL_b_out), .DB_C_acfbba71(DB_C_acfbba71), .ACR_C_fc5559e8(ACR_C_fc5559e8),
    .IR5_D_a37efeb0(IR5_D_a37efeb0), .PHI1(PHI1), .PHI2(PHI2));
  ALU_SETUP alu_setup_1 (
    .NDB_ADD_5826378a(NDB_ADD_5826378a), .ADD_SB06_79b3146b(ADD_SB06_79b3146b),
    .ADD_ADL_d25cdcd8(ADD_ADL_d25cdcd8), .L_DSA_8e87f2a8(L_DSA_8e87f2a8), .INC_SB(alu_setup_1_inc_sb),
    .SR(alu_setup_1_sr), .DB_ADD_49072aec(DB_ADD_49072aec), .L_0_ADD_7d0d5e3b(L_0_ADD_7d0d5e3b),
    .SB_ADD_21cc08e7(SB_ADD_21cc08e7), .ADL_ADD_b3e2e6b8(ADL_ADD_b3e2e6b8), .AND(alu_setup_1_and),
    .ANDS(ANDS), .EORS(EORS), .ORS(ORS), .L_ACIN_e8912140(L_ACIN_e8912140), .SRS(SRS), .SUMS(SUMS),
    .L_DAA_9902be4a(L_DAA_9902be4a), .ADD_SB7_3b72c6f5(ADD_SB7_3b72c6f5), .D56(X56), .D69(X69), .D70(X70),
    .L_ready_2ba3d9e7(L_READY_29998178), .D75(X75), .D76(X76), .D84(X84), .D85(X85), .D86(X86), .D87(X87),
    .D88(X88), .D89(X89), .T0(T0), .T1(T1), .BRK6E(BRK6E), .T5(T5), .T6(T6), .PGX(bus_control_1_pgx),
    .BR3(X93), .L_D_OUT_eaa1b777(L_D_OUT_eaa1b777), .L_C_OUT_e01a0d59(L_C_OUT_e01a0d59),
    .STKOP(regs_control_1_stkop), .PHI1(PHI1), .D26(X26), .D27(X27), .D29(X29), .D30(X30), .D31(X31),
    .D32(X32), .D33(X33), .D34(X34), .D35(X35), .D36(X36), .PHI2(PHI2), .D37(X37), .D38(X38), .D39(X39),
    .D40(X40), .D41(X41), .D42(X42), .D43(X43), .D44(X44), .D45(X45), .D47(X47), .BRFW(branch_logic_1_brfw),
    .D48(X48), .D49(X49), .D50(X50), .D51(X51), .D52(X52), .D53(X53), .D54(X54));
  and and_1 (BR0, X73, ~L_PRDY_7910aae2);  // AND_Gate
  BUS_CONTROL bus_control_1 (
    .L_0_ADH0_8d3f04fb(L_0_ADH0_8d3f04fb), .ADH_ABH_4fac1902(ADH_ABH_4fac1902),
    .DL_DB_4a6f16a8(DL_DB_4a6f16a8), .L_0_ADH17_42b6e0bd(L_0_ADH17_42b6e0bd),
    .SB_AC_692b76aa(SB_AC_692b76aa), .ZTST(bus_control_1_ztst), .ADL_ABL_ccbf1bfb(ADL_ABL_ccbf1bfb),
    .AC_SB_4f3a8e20(AC_SB_4f3a8e20), .SB_DB_92ea0e91(SB_DB_92ea0e91), .AC_DB_7461a43f(AC_DB_7461a43f),
    .PGX(bus_control_1_pgx), .SB_ADH_3fc727a4(SB_ADH_3fc727a4), .DL_ADH_067137e0(DL_ADH_067137e0),
    .DL_ADL_73e48c13(DL_ADL_73e48c13), .D129(X129), .L_0_ADL0_372ea1ce(L_0_ADL0_372ea1ce), .BR2(X80),
    .ACRL2(dispatch_1_acrl2), .D55(X55), .DL_PCH_8d3d82e3(pc_setup_1_dl_pch_8d3d82e3), .BR3(X93),
    .L_ready_2ba3d9e7(L_READY_29998178), .T2(X28), .INC_SB(alu_setup_1_inc_sb), .D45(X45), .BRK6E(BRK6E),
    .D46(X46), .D47(X47), .D48(X48), .D57(X57), .STXY(regs_control_1_stxy), .D101(X101),
    .L_PCH_PCH_45eb8196(pc_setup_1_l_pch_pch_45eb8196), .T0(T0), .T1(T1), .T5(T6), .T6(T5), .D56(X56),
    .D58(X58), .PHI1(PHI1), .D59(X59), .D60(X60), .D61(X61), .D62(X62), .D63(X63), .D64(X64), .D65(X65),
    .D66(X66), .D67(X67), .D68(X68), .PHI2(PHI2), .AND(alu_setup_1_and), .D71(X71), .D72(X72), .D73(BR0),
    .D74(X74), .D79(X79), .STOR(dispatch_1_stor), .D81(X81), .D82(X82), .D84(X84),
    .SBXY(regs_control_1_sbxy), .D89(X89), .D90(X90), .D91(X91), .D83(X83), .D128(X128));
  PC_SETUP pc_setup_1 (
    .PCL_DB_8c5417e4(PCL_DB_8c5417e4), .PCH_DB_4d5eb992(PCH_DB_4d5eb992),
    .PC_DB_528571a6(pc_setup_1_pc_db_528571a6), .PCL_ADL_75837bef(PCL_ADL_75837bef),
    .PCH_ADH_329c7fb7(PCH_ADH_329c7fb7), .PCL_PCL_effd7227(PCL_PCL_effd7227),
    .ADL_PCL_0d330abd(ADL_PCL_0d330abd), .L_ADL_PCL_8a671021(pc_setup_1_l_adl_pcl_8a671021),
    .DL_PCH_8d3d82e3(pc_setup_1_dl_pch_8d3d82e3), .ADH_PCH_413c8ef5(ADH_PCH_413c8ef5),
    .PCH_PCH_e0d1ea0f(PCH_PCH_e0d1ea0f), .L_PCH_PCH_45eb8196(pc_setup_1_l_pch_pch_45eb8196), .D56(X56),
    .D77(X77), .D78(X78), .D83(X83), .D84(X84), .D94(X94), .D95(X95), .D96(X96), .PHI1(PHI1), .D129(X129),
    .L_ready_2ba3d9e7(L_READY_29998178), .BR3(X93), .BR2(X80), .T0(T0), .T1(T1), .BR0(BR0), .PHI2(PHI2));
  DISPATCH dispatch_1 (
    .WR(WR), .T1(T1), .TRES1(TRES1), .L_T0_be2341f9(L_T0_be2341f9), .T0(T0), .T5(T5),
    .L_T1X_cd47d06e(L_T1X_cd47d06e), .L_1_PC_f7ea2184(L_1_PC_f7ea2184), .ACRL2(dispatch_1_acrl2), .T6(T6),
    .TRES2(TRES2), .TRESX(TRESX), .STOR(dispatch_1_stor), .ENDX_Debug(ENDX), .ENDS_Debug(ENDS),
    .L_0_IR_fde7bd13(L_0_IR_fde7bd13), .FETCH(FETCH), .L_ready_2ba3d9e7(L_READY_29998178),
    .L_BRTAKEN_2a78ebe8(branch_logic_1_l_brtaken_2a78ebe8), .L_TWOCYCLE_43089fae(L_TWOCYCLE_43089fae),
    .BRK6E(BRK6E), .L_ADL_PCL_8a671021(pc_setup_1_l_adl_pcl_8a671021),
    .L_IMPLIED_7f832bff(L_IMPLIED_7f832bff), .BR2(X80), .RESP(RESP), .ACR(ACR),
    .DORES(INTERRUPT_RESET_CONTROL_dores), .PC_DB_528571a6(pc_setup_1_pc_db_528571a6), .D91(X91), .D92(X92),
    .PHI1(PHI1), .BR3(X93), .D96(X96), .D97(X97), .D98(X98), .D100(X100), .D101(X101), .D102(X102),
    .D103(X103), .D104(X104), .D105(X105), .PHI2(PHI2), .D106(X106), .D107(X107), .D111(X111), .D122(X122),
    .D123(X123), .D124(X124), .D125(X125), .RDY(RDY), .B_OUT(INTERRUPT_RESET_CONTROL_b_out),
    .BRFW(branch_logic_1_brfw));
  FLAGS_CONTROL flags_control_1 (
    .IR5_I_a8b17eb4(IR5_I_a8b17eb4), .IR5_C_bb157132(IR5_C_bb157132), .IR5_D_a37efeb0(IR5_D_a37efeb0),
    .L_0_V_6d5b0af2(L_0_V_6d5b0af2), .ACR_C_fc5559e8(ACR_C_fc5559e8), .DBZ_Z_805d2a94(DBZ_Z_805d2a94),
    .P_DB_0ea80532(P_DB_0ea80532), .DB_N_4f1ad326(DB_N_4f1ad326), .DB_P_0fe10735(DB_P_0fe10735),
    .DB_C_acfbba71(DB_C_acfbba71), .DB_V_9eaeb3a2(DB_V_9eaeb3a2), .D99(X99), .D108(X108), .D110(X110),
    .D120(X120), .D127(X127), .D107(X107), .PHI2(PHI2), .T6(T6), .D112(X112), .D116(X116), .D117(X117),
    .D118(X118), .D119(X119), .ZTST(bus_control_1_ztst), .D109(X109), .L_ready_2ba3d9e7(L_READY_29998178),
    .SR(alu_setup_1_sr), .D114(X114), .D115(X115), .D98(X98), .D113(X113));
  BRANCH_LOGIC branch_logic_1 (
    .L_BRTAKEN_2a78ebe8(branch_logic_1_l_brtaken_2a78ebe8), .BRFW(branch_logic_1_brfw), .D126(X126),
    .L_C_OUT_e01a0d59(L_C_OUT_e01a0d59), .L_V_OUT_cf6c2405(L_V_OUT_cf6c2405),
    .L_N_OUT_f0a30453(L_N_OUT_f0a30453), .L_Z_OUT_273329d7(L_Z_OUT_273329d7),
    .L_IR5_7bf6fd52(L_IR5_7bf6fd52), .PHI1(PHI1), .PHI2(PHI2), .DB7(DB7), .BR2(X80), .D121(X121));
  EXTENDED_CYCLE_COUNTER extended_cycle_counter_1 (
    .L_T2_2b20ddce(L_T2_2b20ddce), .L_T3_2730c10f(L_T3_2730c10f), .L_T4_1ff9fe8e(L_T4_1ff9fe8e),
    .L_T5_e9d210fb(L_T5_e9d210fb), .TRES2(TRES2), .L_ready_2ba3d9e7(L_READY_29998178), .T1(T1), .PHI1(PHI1),
    .PHI2(PHI2));

  // Other names for the same wires on the sheet: BR2 = X80; BR3 = X93; T2 = X28

  // Notes on the sheet:
  //   BRK5
  //   JSR2
  //   STK2
  //   Branch T0 Skip
  //   Push/pull
endmodule

module D_latch_6baf82dd (
  input  EN,
  input  D,
  output Q,
  output NOT_Q
);

  D_Flip_Flop #(.trigger("high")) d_ff_1 (.D(D), .clk(EN), .Q(Q), .Qn(NOT_Q));  // open: preset, reset
endmodule

module NMI_FF (
  input  L_NMI_153cf1a9,
  input  PHI2,
  output NMIP
);

  wire and_1_out, and_2_out, nor_1_out, nor_2_out, not_1_out;

  not not_1 (not_1_out, L_NMI_153cf1a9);
  and and_1 (and_1_out, not_1_out, PHI2);
  nor nor_1 (nor_1_out, and_2_out, nor_2_out);
  and and_2 (and_2_out, L_NMI_153cf1a9, PHI2);
  nor nor_2 (nor_2_out, nor_1_out, and_1_out);
  not not_2 (NMIP, nor_2_out);
endmodule
module INT_RESET_CONTROL (
  input  PHI1,
  input  PHI2,
  input  BRK5,
  input  L_ready_2ba3d9e7,
  input  RESP,
  input  L_NMIP_e9ae5a44,
  input  BR2,
  input  T0,
  input  L_IRQP_906cd47b,
  input  L_I_OUT_a88ea15a,
  output BRK6E,
  output BRK7,
  output BRK5_RDY,
  output DORES,
  output L_DONMI_539abb0d,
  output B_OUT
);

  wire and_2_out, and_3_out, b_latch1_q, b_latch2_q, brk5_latch_q, brk6_latch1_not_q, brk6_latch2_not_q,
       brk6e_latch_q, brk7_latch_not_q, delay_latch1_not_q, delay_latch2_q, donmi_latch_q, ff1_latch_q,
       ff2_latch_q, nand_1_out, nand_2_out, nand_3_out, nmip_latch_q, nor_1_out, nor_2_out, nor_3_out,
       nor_4_out, nor_5_out, nor_6_out, nor_9_out, not_1_out, not_2_out, not_3_out, not_4_out, or_1_out,
       or_2_out, res_latch1_q, res_latch2_q;

  and and_1 (BRK5_RDY, BRK5, not_1_out);
  not not_1 (not_1_out, L_ready_2ba3d9e7);
  not not_2 (not_2_out, brk5_latch_q);
  D_latch_6baf82dd brk5_latch (.Q(brk5_latch_q), .D(BRK5_RDY), .EN(PHI2));  // open: NOT_Q
  D_latch_6baf82dd res_latch1 (.Q(res_latch1_q), .D(RESP), .EN(PHI2));  // open: NOT_Q
  D_latch_6baf82dd res_latch2 (.Q(res_latch2_q), .D(nor_4_out), .EN(PHI1));  // open: NOT_Q
  D_latch_6baf82dd brk7_latch (.NOT_Q(brk7_latch_not_q), .D(BRK7), .EN(PHI2));  // open: Q
  D_latch_6baf82dd nmip_latch (.Q(nmip_latch_q), .D(L_NMIP_e9ae5a44), .EN(PHI1));  // open: NOT_Q
  D_latch_6baf82dd delay_latch1 (.NOT_Q(delay_latch1_not_q), .D(L_DONMI_539abb0d), .EN(PHI2));  // open: Q
  D_latch_6baf82dd ff1_latch (.Q(ff1_latch_q), .D(L_DONMI_539abb0d), .EN(PHI2));  // open: NOT_Q
  D_latch_6baf82dd brk6e_latch (.Q(brk6e_latch_q), .D(BRK6E), .EN(PHI1));  // open: NOT_Q
  or or_1 (or_1_out, L_IRQP_906cd47b, not_3_out);
  not not_3 (not_3_out, L_I_OUT_a88ea15a);
  D_latch_6baf82dd b_latch2 (.Q(b_latch2_q), .D(nor_9_out), .EN(PHI1));  // open: NOT_Q
  not not_4 (not_4_out, b_latch2_q);
  and and_2 (and_2_out, not_2_out, nand_1_out);
  nand nand_1 (nand_1_out, L_ready_2ba3d9e7, brk6_latch1_not_q);
  nor nor_1 (nor_1_out, res_latch1_q, res_latch2_q);
  nor nor_2 (nor_2_out, nmip_latch_q, nor_6_out);
  D_latch_6baf82dd ff2_latch (.Q(ff2_latch_q), .D(nor_2_out), .EN(PHI2));  // open: NOT_Q
  D_latch_6baf82dd delay_latch2 (.Q(delay_latch2_q), .D(delay_latch1_not_q), .EN(PHI1));  // open: NOT_Q
  nor nor_3 (nor_3_out, ff1_latch_q, brk6e_latch_q);
  nand nand_2 (nand_2_out, or_1_out, L_DONMI_539abb0d);
  and and_3 (and_3_out, nand_3_out, not_4_out);
  D_latch_6baf82dd brk6_latch1 (.NOT_Q(brk6_latch1_not_q), .D(and_2_out), .EN(PHI1));  // open: Q
  nor nor_4 (nor_4_out, nor_1_out, BRK6E);
  nor nor_5 (nor_5_out, brk7_latch_not_q, L_NMIP_e9ae5a44, nor_2_out);
  nor nor_6 (nor_6_out, ff2_latch_q, delay_latch2_q);
  nor nor_7 (L_DONMI_539abb0d, donmi_latch_q, nor_3_out);
  or or_2 (or_2_out, BR2, T0);
  D_latch_6baf82dd b_latch1 (.Q(b_latch1_q), .D(and_3_out), .EN(PHI2));  // open: NOT_Q
  D_latch_6baf82dd brk6_latch2 (.NOT_Q(brk6_latch2_not_q), .D(brk6_latch1_not_q), .EN(PHI2));  // open: Q
  nor nor_8 (BRK7, brk6_latch1_not_q, BRK5_RDY);
  not not_5 (DORES, nor_1_out);
  D_latch_6baf82dd donmi_latch (.Q(donmi_latch_q), .D(nor_5_out), .EN(PHI1));  // open: NOT_Q
  nand nand_3 (nand_3_out, or_2_out, nand_2_out);
  nor nor_9 (nor_9_out, b_latch1_q, BRK6E);
  nor nor_10 (BRK6E, brk6_latch2_not_q, L_ready_2ba3d9e7);
  nor nor_11 (B_OUT, DORES, nor_9_out);

  // Notes on the sheet:
  //   /NMIP
  //   /IRQP
  //   INTERRUPT CYCLE 6-7
  //   BRK_FF
  //   RESET FLIP/FLOP
  //   RES_FF
  //   NMI EDGE DETECT
  //   NMI_FF1
  //   INTERRUPT CHECK
  //   BR2
  //   T0
  //   B FLAG
  //   B_FF
  //   NMI_FF2
  //   /DONMI
  //   /DONMI
endmodule

module INT_VECTOR (
  input  PHI2,
  input  BRK5_RDY,
  input  BRK7,
  input  DORES,
  input  L_DONMI_539abb0d,
  output L_0_ADL0_372ea1ce,
  output L_0_ADL1_1828b789,
  output L_0_ADL2_a1d2ebaa
);

  wire nor_1_out, nor_2_out, not_1_out, not_2_out, not_3_out, zadl2_latch_not_q;

  not not_1 (not_1_out, DORES);
  not not_2 (not_2_out, BRK5_RDY);
  nor nor_1 (nor_1_out, BRK7, not_1_out);
  not not_3 (not_3_out, nor_1_out);
  nor nor_2 (nor_2_out, BRK7, DORES, L_DONMI_539abb0d);
  D_latch_6baf82dd zadl0_latch (.NOT_Q(L_0_ADL0_372ea1ce), .D(not_2_out), .EN(PHI2));  // open: Q
  D_latch_6baf82dd zadl1_latch (.NOT_Q(L_0_ADL1_1828b789), .D(not_3_out), .EN(PHI2));  // open: Q
  D_latch_6baf82dd zadl2_latch (.NOT_Q(zadl2_latch_not_q), .D(nor_2_out), .EN(PHI2));  // open: Q
  not not_4 (L_0_ADL2_a1d2ebaa, zadl2_latch_not_q);

  // Notes on the sheet:
  //   FFFA:NMI, 1010
  //   FFFC:RESET, 1100
  //   FFFE:IRQ/BRK, 1110
endmodule

module REGS_CONTROL (
  input  PHI1,
  input  PHI2,
  input  STOR,
  input  D0,
  input  D1,
  input  D2,
  input  D3,
  input  D4,
  input  D5,
  input  D6,
  input  D7,
  input  D8,
  input  D9,
  input  D10,
  input  D11,
  input  D12,
  input  D13,
  input  D14,
  input  D15,
  input  D16,
  input  D17,
  input  D18,
  input  D19,
  input  D20,
  input  D21,
  input  D22,
  input  D23,
  input  D24,
  input  D25,
  input  D26,
  input  D48,
  input  L_ready_2ba3d9e7,
  input  D35,
  output Y_SB_981fc62c,
  output STXY,
  output X_SB_50e8fb84,
  output S_SB_c8f0deaa,
  output SB_X_a4a389b1,
  output SBXY,
  output SB_Y_f952d371,
  output SB_S_e7e7b943,
  output S_S_0e77937e,
  output STKOP,
  output S_ADL_299349f9
);

  wire and_1_out, and_2_out, and_3_out, and_4_out, and_5_out, and_6_out, and_7_out, nor_1_out, nor_2_out,
       nor_3_out, nor_4_out, nor_5_out, nor_6_out, nor_8_out, nor_9_out, nor_11_out, nor_12_out, nor_13_out,
       nor_14_out, nor_15_out, nor_16_out, not_1_out, not_2_out, not_3_out, not_4_out, nready_latch_not_q,
       nready_latch_q, sadl_latch_not_q, sbs_latch_q, sbx_latch_q, sby_latch_q, ss_latch_q, ssb_latch_not_q,
       xsb_latch_q, ysb_latch_q;

  and and_1 (and_1_out, D6, D7);
  and and_2 (and_2_out, D6, not_1_out);
  not not_1 (not_1_out, D7);
  nor nor_1 (nor_1_out, D14, D15, D16);
  not not_2 (not_2_out, D17);
  nor nor_2 (nor_2_out, D18, D19, D20);
  not not_3 (not_3_out, D48);
  nor nor_3 (nor_3_out, D21, D22, D23, D24, D25, D26);
  and and_3 (and_3_out, STOR, D0);
  and and_4 (and_4_out, STOR, D12);
  D_latch_6baf82dd nready_latch (.Q(nready_latch_q), .NOT_Q(nready_latch_not_q), .D(L_ready_2ba3d9e7), .EN(PHI1));
  nor nor_4 (nor_4_out, not_3_out, L_ready_2ba3d9e7);
  nor nor_5 (nor_5_out, D1, D2, D3, D4, D5, and_1_out, and_3_out);
  nor nor_6 (nor_6_out, and_4_out, and_2_out, D8, D9, D10, D11, D13);
  and and_5 (and_5_out, D21, nready_latch_not_q);
  nor nor_7 (STKOP, nor_3_out, nready_latch_q);
  and and_6 (and_6_out, STOR, D0);
  and and_7 (and_7_out, STOR, D12);
  nand nand_1 (SBXY, nor_1_out, nor_2_out);
  nor nor_8 (nor_8_out, D13, nor_4_out, STKOP);
  nor nor_9 (nor_9_out, and_5_out, D35);
  not not_4 (not_4_out, nor_8_out);
  D_latch_6baf82dd ysb_latch (.Q(ysb_latch_q), .D(nor_5_out), .EN(PHI2));  // open: NOT_Q
  nor nor_10 (STXY, and_6_out, and_7_out);
  D_latch_6baf82dd xsb_latch (.Q(xsb_latch_q), .D(nor_6_out), .EN(PHI2));  // open: NOT_Q
  D_latch_6baf82dd ssb_latch (.NOT_Q(ssb_latch_not_q), .D(not_2_out), .EN(PHI2));  // open: Q
  D_latch_6baf82dd sbx_latch (.Q(sbx_latch_q), .D(nor_1_out), .EN(PHI2));  // open: NOT_Q
  D_latch_6baf82dd sby_latch (.Q(sby_latch_q), .D(nor_2_out), .EN(PHI2));  // open: NOT_Q
  D_latch_6baf82dd sbs_latch (.Q(sbs_latch_q), .D(nor_8_out), .EN(PHI2));  // open: NOT_Q
  D_latch_6baf82dd ss_latch (.Q(ss_latch_q), .D(not_4_out), .EN(PHI2));  // open: NOT_Q
  D_latch_6baf82dd sadl_latch (.NOT_Q(sadl_latch_not_q), .D(nor_9_out), .EN(PHI2));  // open: Q
  nor nor_11 (nor_11_out, ysb_latch_q, PHI2);
  buf buffer_1 (Y_SB_981fc62c, nor_11_out);
  nor nor_12 (nor_12_out, xsb_latch_q, PHI2);
  buf buffer_2 (X_SB_50e8fb84, nor_12_out);
  buf buffer_3 (S_SB_c8f0deaa, ssb_latch_not_q);
  nor nor_13 (nor_13_out, sbx_latch_q, PHI2);
  buf buffer_4 (SB_X_a4a389b1, nor_13_out);
  nor nor_14 (nor_14_out, sby_latch_q, PHI2);
  buf buffer_5 (SB_Y_f952d371, nor_14_out);
  nor nor_15 (nor_15_out, sbs_latch_q, PHI2);
  buf buffer_6 (SB_S_e7e7b943, nor_15_out);
  nor nor_16 (nor_16_out, ss_latch_q, PHI2);
  buf buffer_7 (S_S_0e77937e, nor_16_out);
  buf buffer_8 (S_ADL_299349f9, sadl_latch_not_q);

  // Notes on the sheet:
  //   JSR2
  //   STK2
  //   TXS
  //   #SB/X
  //   #S/SB
  //   #SB/Y
  //   STOR
  //   STOR
  //   STKOP
  //   #Y/SB
  //   #X/SB
  //   #S/SB
  //   SBXY
  //   #SB/S
  //   #S/ADL
endmodule

module EXTENDED_CYCLE_COUNTER (
  input  PHI1,
  input  PHI2,
  input  TRES2,
  input  L_ready_2ba3d9e7,
  input  T1,
  output L_T2_2b20ddce,
  output L_T3_2730c10f,
  output L_T4_1ff9fe8e,
  output L_T5_e9d210fb
);

  wire multiplexer_1_out, multiplexer_2_out, multiplexer_3_out, multiplexer_4_out, nor_1_out, nor_2_out,
       nor_3_out, nor_4_out, t1_latch_not_q, t2_latch1_q, t2_latch2_not_q, t3_latch1_q, t3_latch2_not_q,
       t4_latch1_q, t4_latch2_not_q, t5_latch1_q, t5_latch2_not_q;

  D_latch_6baf82dd t1_latch (.NOT_Q(t1_latch_not_q), .D(T1), .EN(PHI2));  // open: Q
  Multiplexer multiplexer_1 (
    .in0(t1_latch_not_q), .in1(t2_latch2_not_q), .out(multiplexer_1_out), .sel(L_ready_2ba3d9e7));
  Multiplexer multiplexer_2 (
    .in0(t2_latch2_not_q), .in1(t3_latch2_not_q), .out(multiplexer_2_out), .sel(L_ready_2ba3d9e7));
  Multiplexer multiplexer_3 (
    .in0(t3_latch2_not_q), .in1(t4_latch2_not_q), .out(multiplexer_3_out), .sel(L_ready_2ba3d9e7));
  Multiplexer multiplexer_4 (
    .in0(t4_latch2_not_q), .in1(t5_latch2_not_q), .out(multiplexer_4_out), .sel(L_ready_2ba3d9e7));
  nor nor_1 (nor_1_out, TRES2, t2_latch1_q);
  nor nor_2 (nor_2_out, TRES2, t3_latch1_q);
  nor nor_3 (nor_3_out, TRES2, t4_latch1_q);
  nor nor_4 (nor_4_out, TRES2, t5_latch1_q);
  D_latch_6baf82dd t2_latch2 (.NOT_Q(t2_latch2_not_q), .D(nor_1_out), .EN(PHI2));  // open: Q
  D_latch_6baf82dd t2_latch1 (.Q(t2_latch1_q), .D(multiplexer_1_out), .EN(PHI1));  // open: NOT_Q
  D_latch_6baf82dd t3_latch2 (.NOT_Q(t3_latch2_not_q), .D(nor_2_out), .EN(PHI2));  // open: Q
  D_latch_6baf82dd t3_latch1 (.Q(t3_latch1_q), .D(multiplexer_2_out), .EN(PHI1));  // open: NOT_Q
  D_latch_6baf82dd t4_latch2 (.NOT_Q(t4_latch2_not_q), .D(nor_3_out), .EN(PHI2));  // open: Q
  D_latch_6baf82dd t4_latch1 (.Q(t4_latch1_q), .D(multiplexer_3_out), .EN(PHI1));  // open: NOT_Q
  D_latch_6baf82dd t5_latch2 (.NOT_Q(t5_latch2_not_q), .D(nor_4_out), .EN(PHI2));  // open: Q
  D_latch_6baf82dd t5_latch1 (.Q(t5_latch1_q), .D(multiplexer_4_out), .EN(PHI1));  // open: NOT_Q
  not not_1 (L_T2_2b20ddce, nor_1_out);
  not not_2 (L_T3_2730c10f, nor_2_out);
  not not_3 (L_T4_1ff9fe8e, nor_3_out);
  not not_4 (L_T5_e9d210fb, nor_4_out);
endmodule

module ALU_SETUP (
  input  PHI1,
  input  PHI2,
  input  BRFW,
  input  L_ready_2ba3d9e7,
  input  BRK6E,
  input  STKOP,
  input  D26,
  input  D27,
  input  D29,
  input  D30,
  input  D31,
  input  D32,
  input  D33,
  input  D34,
  input  D35,
  input  D36,
  input  D37,
  input  D38,
  input  D39,
  input  D40,
  input  D41,
  input  D42,
  input  D43,
  input  D44,
  input  D45,
  input  D47,
  input  D48,
  input  D49,
  input  D50,
  input  D51,
  input  D52,
  input  D53,
  input  D54,
  input  D56,
  input  D69,
  input  D70,
  input  D75,
  input  D76,
  input  D84,
  input  D85,
  input  D86,
  input  D87,
  input  D88,
  input  D89,
  input  T0,
  input  T1,
  input  T5,
  input  T6,
  input  PGX,
  input  BR3,
  input  L_D_OUT_eaa1b777,
  input  L_C_OUT_e01a0d59,
  output NDB_ADD_5826378a,
  output DB_ADD_49072aec,
  output L_0_ADD_7d0d5e3b,
  output SB_ADD_21cc08e7,
  output ADL_ADD_b3e2e6b8,
  output AND,
  output ANDS,
  output EORS,
  output ORS,
  output L_ACIN_e8912140,
  output SRS,
  output SUMS,
  output L_DAA_9902be4a,
  output ADD_SB7_3b72c6f5,
  output ADD_SB06_79b3146b,
  output ADD_ADL_d25cdcd8,
  output L_DSA_8e87f2a8,
  output INC_SB,
  output SR
);

  wire acin_latch1_q, acin_latch2_q, acin_latch3_q, acin_latch4_q, acin_latch5_not_q,
       add_sb7_inst_l_add_sb7_42ccbd8d, addadl_latch_not_q, addsb06_latch_not_q, addsb7_latch_q,
       adladd_latch_q, and_1_out, and_2_out, and_3_out, ands_latch1_not_q, ands_latch2_not_q,
       daa_latch1_not_q, daa_latch2_not_q, dbadd_latch_q, dsa_latch1_not_q, eors_latch1_not_q,
       eors_latch2_not_q, nand_1_out, nand_2_out, nand_3_out, nand_4_out, nand_5_out, nand_6_out,
       ndbadd_latch_q, nor_1_out, nor_2_out, nor_3_out, nor_4_out, nor_5_out, nor_6_out, nor_7_out,
       nor_8_out, nor_9_out, nor_10_out, nor_11_out, nor_12_out, nor_13_out, nor_14_out, nor_15_out,
       nor_16_out, nor_17_out, nor_18_out, nor_19_out, nor_20_out, nor_21_out, nor_22_out, nor_23_out,
       not_1_out, not_2_out, not_4_out, not_5_out, not_6_out, not_9_out, not_10_out, not_11_out, not_12_out,
       not_13_out, not_14_out, not_15_out, or_1_out, or_2_out, ors_latch1_not_q, ors_latch2_not_q,
       sbadd_latch_q, srs_latch1_not_q, srs_latch2_not_q, sums_latch1_not_q, sums_latch2_not_q, zadd_latch_q;

  not not_1 (not_1_out, D34);
  not not_2 (not_2_out, L_D_OUT_eaa1b777);
  nor nor_1 (nor_1_out, D32, L_ready_2ba3d9e7);
  and and_1 (and_1_out, D33, not_1_out);
  and and_2 (and_2_out, T5, D44);
  or or_1 (or_1_out, D52, D53);
  nor nor_2 (nor_2_out, D69, D70);
  not not_3 (AND, nor_2_out);
  and and_3 (and_3_out, D76, T5);
  not not_4 (not_4_out, D27);
  not not_5 (not_5_out, nor_1_out);
  nor nor_3 (nor_3_out, and_1_out, D35, D36, D37, D38, D39, L_ready_2ba3d9e7);
  nor nor_4 (nor_4_out, D39, D40, D41, D42, D43, and_2_out);
  not not_6 (not_6_out, BR3);
  nor nor_5 (nor_5_out, D75, and_3_out);
  not not_7 (SR, nor_5_out);
  nor nor_6 (nor_6_out, D84, D85, D86, D87, D88, D89, D26);
  not not_8 (INC_SB, nor_4_out);
  nor nor_7 (nor_7_out, not_6_out, BRFW);
  nor nor_8 (nor_8_out, T0, T5);
  not not_9 (not_9_out, D47);
  nor nor_9 (nor_9_out, D49, D50, nor_7_out);
  not not_10 (not_10_out, nor_9_out);
  nor nor_10 (nor_10_out, L_C_OUT_e01a0d59, nor_8_out);
  nor nor_11 (nor_11_out, STKOP, D30, D31, D45, D48, INC_SB, D47, BRK6E, L_ready_2ba3d9e7);
  nor nor_12 (nor_12_out, nor_3_out, not_9_out);
  nand nand_1 (nand_1_out, nor_10_out, or_1_out);
  not not_11 (not_11_out, D54);
  nand nand_2 (nand_2_out, nand_1_out, not_11_out);
  nand nand_3 (nand_3_out, D52, not_2_out);
  nor nor_13 (nor_13_out, nor_6_out, PGX);
  nor nor_14 (nor_14_out, nand_3_out, D51);
  nand nand_4 (nand_4_out, D51, not_2_out);
  or or_2 (or_2_out, not_10_out, D56, D51);
  D_latch_6baf82dd acin_latch1 (.Q(acin_latch1_q), .D(nor_12_out), .EN(PHI2));  // open: NOT_Q
  D_latch_6baf82dd acin_latch2 (.Q(acin_latch2_q), .D(INC_SB), .EN(PHI2));  // open: NOT_Q
  D_latch_6baf82dd acin_latch3 (.Q(acin_latch3_q), .D(not_10_out), .EN(PHI2));  // open: NOT_Q
  D_latch_6baf82dd acin_latch4 (.Q(acin_latch4_q), .D(nand_2_out), .EN(PHI2));  // open: NOT_Q
  not not_12 (not_12_out, nor_13_out);
  not not_13 (not_13_out, nor_14_out);
  not not_14 (not_14_out, L_ready_2ba3d9e7);
  nor nor_15 (nor_15_out, acin_latch1_q, acin_latch2_q, acin_latch3_q, acin_latch4_q);
  nand nand_5 (nand_5_out, or_2_out, not_14_out);
  ADD_SB7 add_sb7_inst (
    .L_ADD_SB7_42ccbd8d(add_sb7_inst_l_add_sb7_42ccbd8d), .PHI2(PHI2), .L_C_OUT_e01a0d59(L_C_OUT_e01a0d59),
    .L_ready_2ba3d9e7(L_ready_2ba3d9e7), .SR(SR), .L_ROR_e72329fe(not_4_out), .PHI1(PHI1));
  nor nor_16 (nor_16_out, T6, PGX);
  nand nand_6 (nand_6_out, nand_5_out, nor_3_out);
  nor nor_17 (nor_17_out, AND, D29, not_5_out, SR);
  nor nor_18 (nor_18_out, nor_16_out, add_sb7_inst_l_add_sb7_42ccbd8d);
  not not_15 (not_15_out, nor_11_out);
  D_latch_6baf82dd ndbadd_latch (.Q(ndbadd_latch_q), .D(nand_5_out), .EN(PHI2));  // open: NOT_Q
  D_latch_6baf82dd dbadd_latch (.Q(dbadd_latch_q), .D(nand_6_out), .EN(PHI2));  // open: NOT_Q
  D_latch_6baf82dd zadd_latch (.Q(zadd_latch_q), .D(nor_11_out), .EN(PHI2));  // open: NOT_Q
  D_latch_6baf82dd sbadd_latch (.Q(sbadd_latch_q), .D(not_15_out), .EN(PHI2));  // open: NOT_Q
  D_latch_6baf82dd adladd_latch (.Q(adladd_latch_q), .D(nor_3_out), .EN(PHI2));  // open: NOT_Q
  D_latch_6baf82dd ands_latch1 (.NOT_Q(ands_latch1_not_q), .D(AND), .EN(PHI2));  // open: Q
  D_latch_6baf82dd eors_latch1 (.NOT_Q(eors_latch1_not_q), .D(D29), .EN(PHI2));  // open: Q
  D_latch_6baf82dd ors_latch1 (.NOT_Q(ors_latch1_not_q), .D(not_5_out), .EN(PHI2));  // open: Q
  D_latch_6baf82dd srs_latch1 (.NOT_Q(srs_latch1_not_q), .D(SR), .EN(PHI2));  // open: Q
  D_latch_6baf82dd sums_latch1 (.NOT_Q(sums_latch1_not_q), .D(nor_17_out), .EN(PHI2));  // open: Q
  D_latch_6baf82dd daa_latch1 (.NOT_Q(daa_latch1_not_q), .D(not_13_out), .EN(PHI2));  // open: Q
  D_latch_6baf82dd addsb7_latch (.Q(addsb7_latch_q), .D(nor_18_out), .EN(PHI2));  // open: NOT_Q
  D_latch_6baf82dd addsb06_latch (.NOT_Q(addsb06_latch_not_q), .D(nor_16_out), .EN(PHI2));  // open: Q
  D_latch_6baf82dd addadl_latch (.NOT_Q(addadl_latch_not_q), .D(not_12_out), .EN(PHI2));  // open: Q
  D_latch_6baf82dd dsa_latch1 (.NOT_Q(dsa_latch1_not_q), .D(nand_4_out), .EN(PHI2));  // open: Q
  nor nor_19 (nor_19_out, ndbadd_latch_q, PHI2);
  nor nor_20 (nor_20_out, dbadd_latch_q, PHI2);
  nor nor_21 (nor_21_out, zadd_latch_q, PHI2);
  nor nor_22 (nor_22_out, sbadd_latch_q, PHI2);
  nor nor_23 (nor_23_out, adladd_latch_q, PHI2);
  D_latch_6baf82dd ands_latch2 (.NOT_Q(ands_latch2_not_q), .D(ands_latch1_not_q), .EN(PHI1));  // open: Q
  buf buffer_1 (ANDS, ands_latch2_not_q);
  D_latch_6baf82dd eors_latch2 (.NOT_Q(eors_latch2_not_q), .D(eors_latch1_not_q), .EN(PHI1));  // open: Q
  buf buffer_2 (EORS, eors_latch2_not_q);
  D_latch_6baf82dd ors_latch2 (.NOT_Q(ors_latch2_not_q), .D(ors_latch1_not_q), .EN(PHI1));  // open: Q
  buf buffer_3 (ORS, ors_latch2_not_q);
  D_latch_6baf82dd acin_latch5 (.NOT_Q(acin_latch5_not_q), .D(nor_15_out), .EN(PHI1));  // open: Q
  not not_16 (L_ACIN_e8912140, acin_latch5_not_q);
  D_latch_6baf82dd srs_latch2 (.NOT_Q(srs_latch2_not_q), .D(srs_latch1_not_q), .EN(PHI1));  // open: Q
  buf buffer_4 (SRS, srs_latch2_not_q);
  D_latch_6baf82dd sums_latch2 (.NOT_Q(sums_latch2_not_q), .D(sums_latch1_not_q), .EN(PHI1));  // open: Q
  buf buffer_5 (SUMS, sums_latch2_not_q);
  D_latch_6baf82dd daa_latch2 (.NOT_Q(daa_latch2_not_q), .D(daa_latch1_not_q), .EN(PHI1));  // open: Q
  buf buffer_6 (L_DAA_9902be4a, daa_latch2_not_q);
  buf buffer_7 (ADD_SB7_3b72c6f5, addsb7_latch_q);
  buf buffer_8 (ADD_SB06_79b3146b, addsb06_latch_not_q);
  buf buffer_9 (ADD_ADL_d25cdcd8, addadl_latch_not_q);
  D_latch_6baf82dd dsa_latch2 (.NOT_Q(L_DSA_8e87f2a8), .D(dsa_latch1_not_q), .EN(PHI1));  // open: Q
  buf buffer_10 (NDB_ADD_5826378a, nor_19_out);
  buf buffer_11 (DB_ADD_49072aec, nor_20_out);
  buf buffer_12 (L_0_ADD_7d0d5e3b, nor_21_out);
  buf buffer_13 (SB_ADD_21cc08e7, nor_22_out);
  buf buffer_14 (ADL_ADD_b3e2e6b8, nor_23_out);

  // Other names for the same wires on the sheet: JSR_5_22e7185b = D56; RTI_5_45a526a8 = D26; RTS_5_f937778f = D84;
  //   SBC0 = D51

  // Notes on the sheet:
  //   ROR
  //   EOR
  //   STK2
  //   RET
  //   JSR2
  //   D_OUT
  //   OR
  //   NOADL
  //   #ADL/ADD
  //   BRX
  //   SB/ADD
  //   CSET
  //   PGX
  //   /ACIN
  //   #NDB/ADD
  //   #ADD/SB7
  //   #ADD/SB06
  //   #ADL/ADD
  //   care!
endmodule

module BRANCH_LOGIC (
  input  L_IR5_7bf6fd52,
  input  D121,
  input  D126,
  input  L_C_OUT_e01a0d59,
  input  L_V_OUT_cf6c2405,
  input  L_N_OUT_f0a30453,
  input  L_Z_OUT_273329d7,
  input  PHI1,
  input  PHI2,
  input  DB7,
  input  BR2,
  output L_BRTAKEN_2a78ebe8,
  output BRFW
);

  wire br2_latch_q, brfw_latch1_not_q, brfw_latch2_q, multiplexer_1_out, nor_1_out, nor_2_out, nor_3_out,
       nor_4_out, nor_5_out, not_1_out, not_2_out, not_3_out, not_4_out, not_5_out, not_6_out;

  not not_1 (not_1_out, D121);
  not not_2 (not_2_out, D126);
  not not_3 (not_3_out, D126);
  not not_4 (not_4_out, D121);
  not not_5 (not_5_out, DB7);
  D_latch_6baf82dd br2_latch (.Q(br2_latch_q), .D(BR2), .EN(PHI2));  // open: NOT_Q
  D_latch_6baf82dd brfw_latch2 (.Q(brfw_latch2_q), .D(brfw_latch1_not_q), .EN(PHI2));  // open: NOT_Q
  nor nor_1 (nor_1_out, L_C_OUT_e01a0d59, D126, not_1_out);
  nor nor_2 (nor_2_out, L_V_OUT_cf6c2405, D121, not_2_out);
  nor nor_3 (nor_3_out, L_N_OUT_f0a30453, not_3_out, not_4_out);
  nor nor_4 (nor_4_out, D126, D121, L_Z_OUT_273329d7);
  nor nor_5 (nor_5_out, nor_1_out, nor_2_out, nor_3_out, nor_4_out);
  Multiplexer multiplexer_1 (.in0(brfw_latch2_q), .in1(not_5_out), .out(multiplexer_1_out), .sel(br2_latch_q));
  xor xor_1 (L_BRTAKEN_2a78ebe8, L_IR5_7bf6fd52, nor_5_out);
  not not_6 (not_6_out, multiplexer_1_out);
  D_latch_6baf82dd brfw_latch1 (.NOT_Q(brfw_latch1_not_q), .D(not_6_out), .EN(PHI1));  // open: Q
  not not_7 (BRFW, brfw_latch1_not_q);

  // Notes on the sheet:
  //   /IR6
  //   /IR7
  //   BRFW_FF
endmodule

// PROGRAM COUNTER SETUP
module PC_SETUP (
  input  PHI1,
  input  PHI2,
  input  D56,
  input  D77,
  input  D78,
  input  D83,
  input  D84,
  input  D94,
  input  D95,
  input  D96,
  input  D129,
  input  L_ready_2ba3d9e7,
  input  BR3,
  input  BR2,
  input  T0,
  input  T1,
  input  BR0,
  output PCL_DB_8c5417e4,
  output PCH_DB_4d5eb992,
  output PC_DB_528571a6,
  output PCL_ADL_75837bef,
  output PCH_ADH_329c7fb7,
  output PCL_PCL_effd7227,
  output ADL_PCL_0d330abd,
  output L_ADL_PCL_8a671021,
  output DL_PCH_8d3d82e3,
  output ADH_PCH_413c8ef5,
  output PCH_PCH_e0d1ea0f,
  output L_PCH_PCH_45eb8196
);

  wire adh_pch_latch_q, adl_pcl_latch_q, and_1_out, and_2_out, nor_1_out, nor_2_out, nor_3_out, nor_4_out,
       nor_5_out, nor_8_out, nor_9_out, nor_10_out, nor_11_out, nor_12_out, nor_13_out, nor_14_out,
       nor_15_out, not_1_out, not_2_out, not_3_out, not_5_out, nready_latch_q, pch_adh_latch_not_q,
       pch_db_latch1_q, pch_db_latch2_not_q, pch_pch_latch_q, pcl_adl_latch_not_q, pcl_db_latch1_not_q,
       pcl_db_latch2_not_q, pcl_pcl_latch_q;

  nor nor_1 (nor_1_out, D77, D78);
  and and_1 (and_1_out, D83, ~D129);  // AND_Gate
  nor nor_2 (nor_2_out, D94, D95, D96);
  D_latch_6baf82dd pch_db_latch1 (.Q(pch_db_latch1_q), .D(nor_1_out), .EN(PHI2));  // open: NOT_Q
  D_latch_6baf82dd nready_latch (.Q(nready_latch_q), .D(L_ready_2ba3d9e7), .EN(PHI1));  // open: NOT_Q
  nor nor_3 (nor_3_out, pch_db_latch1_q, L_ready_2ba3d9e7);
  nor nor_4 (nor_4_out, nor_2_out, nready_latch_q);
  not not_1 (not_1_out, nready_latch_q);
  not not_2 (not_2_out, T0);
  nor nor_5 (nor_5_out, nor_4_out, not_2_out);
  not not_3 (not_3_out, nor_8_out);
  and and_2 (and_2_out, not_1_out, BR3);
  nor nor_6 (DL_PCH_8d3d82e3, not_2_out, nor_2_out);
  D_latch_6baf82dd pcl_db_latch1 (.NOT_Q(pcl_db_latch1_not_q), .D(nor_3_out), .EN(PHI1));  // open: Q
  nor nor_7 (L_ADL_PCL_8a671021, not_3_out, D84, T0, and_2_out);
  nand nand_1 (PC_DB_528571a6, pcl_db_latch1_not_q, nor_1_out);
  nor nor_8 (nor_8_out, T1, BR2);
  nor nor_9 (nor_9_out, D84, and_1_out, T0, T1, BR2, BR3);
  nor nor_10 (nor_10_out, nor_8_out, DL_PCH_8d3d82e3, BR0);
  not not_4 (L_PCH_PCH_45eb8196, nor_9_out);
  nor nor_11 (nor_11_out, nor_10_out, BR3);
  not not_5 (not_5_out, L_ADL_PCL_8a671021);
  D_latch_6baf82dd pcl_db_latch2 (.NOT_Q(pcl_db_latch2_not_q), .D(pcl_db_latch1_not_q), .EN(PHI2));  // open: Q
  D_latch_6baf82dd pch_db_latch2 (.NOT_Q(pch_db_latch2_not_q), .D(nor_1_out), .EN(PHI2));  // open: Q
  D_latch_6baf82dd pcl_adl_latch (.NOT_Q(pcl_adl_latch_not_q), .D(nor_8_out), .EN(PHI2));  // open: Q
  D_latch_6baf82dd pch_adh_latch (.NOT_Q(pch_adh_latch_not_q), .D(nor_11_out), .EN(PHI2));  // open: Q
  D_latch_6baf82dd pcl_pcl_latch (.Q(pcl_pcl_latch_q), .D(not_5_out), .EN(PHI2));  // open: NOT_Q
  D_latch_6baf82dd adl_pcl_latch (.Q(adl_pcl_latch_q), .D(L_ADL_PCL_8a671021), .EN(PHI2));  // open: NOT_Q
  D_latch_6baf82dd adh_pch_latch (.Q(adh_pch_latch_q), .D(nor_9_out), .EN(PHI2));  // open: NOT_Q
  D_latch_6baf82dd pch_pch_latch (.Q(pch_pch_latch_q), .D(L_PCH_PCH_45eb8196), .EN(PHI2));  // open: NOT_Q
  nor nor_12 (nor_12_out, pcl_pcl_latch_q, PHI2);
  nor nor_13 (nor_13_out, adl_pcl_latch_q, PHI2);
  nor nor_14 (nor_14_out, adh_pch_latch_q, PHI2);
  nor nor_15 (nor_15_out, pch_pch_latch_q, PHI2);
  buf buffer_1 (PCL_DB_8c5417e4, pcl_db_latch2_not_q);
  buf buffer_2 (PCH_DB_4d5eb992, pch_db_latch2_not_q);
  buf buffer_3 (PCL_ADL_75837bef, pcl_adl_latch_not_q);
  buf buffer_4 (PCH_ADH_329c7fb7, pch_adh_latch_not_q);
  buf buffer_5 (PCL_PCL_effd7227, nor_12_out);
  buf buffer_6 (ADL_PCL_0d330abd, nor_13_out);
  buf buffer_7 (ADH_PCH_413c8ef5, nor_14_out);
  buf buffer_8 (PCH_PCH_e0d1ea0f, nor_15_out);

  // Other names for the same wires on the sheet: RTS_5_f937778f = D84

  // Notes on the sheet:
  //   JRS/5
  //   Push/pull
  //   JB
  //   #PCH/DB
  //   ABS/2
  //   DL/PCH
  //   #PCL/DB
  //   PC/DB
  //   DL/PCH
  //   #PCL/ADL
  //   #ADL/PCL
  //   #ADH/PCH
  //   8
endmodule

module DISPATCH (
  input  PHI1,
  input  PHI2,
  input  BRK6E,
  input  BR2,
  input  RESP,
  input  ACR,
  input  DORES,
  input  PC_DB_528571a6,
  input  D91,
  input  D92,
  input  BR3,
  input  D96,
  input  D97,
  input  D98,
  input  D100,
  input  D101,
  input  D102,
  input  D103,
  input  D104,
  input  D105,
  input  D106,
  input  D107,
  input  D111,
  input  D122,
  input  D123,
  input  D124,
  input  D125,
  input  RDY,
  input  B_OUT,
  input  BRFW,
  input  L_BRTAKEN_2a78ebe8,
  input  L_TWOCYCLE_43089fae,
  input  L_ADL_PCL_8a671021,
  input  L_IMPLIED_7f832bff,
  output ACRL2,
  output T5,
  output T6,
  output TRES2,
  output TRESX,
  output STOR,
  output ENDX_Debug,
  output ENDS_Debug,
  output L_0_IR_fde7bd13,
  output FETCH,
  output L_ready_2ba3d9e7,
  output WR,
  output T1,
  output TRES1,
  output L_T0_be2341f9,
  output T0,
  output L_T1X_cd47d06e,
  output L_1_PC_f7ea2184
);

  wire acr_latch1_not_q, and_1_out, and_2_out, and_3_out, and_4_out, and_5_out, and_6_out, br_latch1_q,
       br_latch2_not_q, comp_latch1_q, comp_latch2_q, comp_latch3_q, ends_latch1_q, ends_latch2_q,
       fetch_latch_not_q, ipc_latch1_q, ipc_latch2_q, ipc_latch3_q, L_MemOP_614ba69e, L_SHIFT_b19c62b1,
       multiplexer_1_out, nand_1_out, nand_2_out, nor_1_out, nor_4_out, nor_5_out, nor_6_out, nor_7_out,
       nor_8_out, nor_9_out, nor_10_out, nor_11_out, nor_12_out, nor_13_out, nor_16_out, nor_17_out,
       nor_18_out, nor_19_out, nor_20_out, nor_21_out, nor_23_out, nor_24_out, nor_25_out, nor_26_out,
       nor_28_out, nor_29_out, nor_30_out, nor_32_out, not_1_out, not_2_out, not_3_out, not_4_out, not_5_out,
       not_6_out, not_7_out, not_8_out, not_9_out, not_10_out, not_11_out, not_12_out, NotReadyPhi1,
       nready_latch_q, or_1_out, rdydelay_latch1_not_q, ready_latch1_not_q, ready_latch2_q, step_latch1_q,
       step_latch2_q, t0_latch_q, t1x_latch_q, t5_latch2_q, t6_latch1_not_q, t6_latch2_not_q, t56_latch_q,
       tresx_latch1_q, tresx_latch2_not_q, wr_latch_q, xor_1_out;

  nor nor_1 (nor_1_out, D91, D92);
  not not_1 (not_1_out, D97);
  nor nor_2 (L_SHIFT_b19c62b1, D106, D107);
  nor nor_3 (L_MemOP_614ba69e, D111, D125);
  nor nor_4 (nor_4_out, BR2, BR3);
  not not_2 (not_2_out, ACR);
  not not_3 (not_3_out, NotReadyPhi1);
  nor nor_5 (nor_5_out, D100, D101, D102, D103, D104, D105);
  not not_4 (not_4_out, nor_5_out);
  not not_5 (not_5_out, nor_4_out);
  not not_6 (not_6_out, L_IMPLIED_7f832bff);
  and and_1 (and_1_out, not_2_out, not_3_out);
  nor nor_6 (nor_6_out, not_3_out, ACRL2);
  and and_2 (and_2_out, L_BRTAKEN_2a78ebe8, BR2);
  not not_7 (not_7_out, BR3);
  and and_3 (and_3_out, L_BRTAKEN_2a78ebe8, BR2);
  nor nor_7 (nor_7_out, L_ADL_PCL_8a671021, not_5_out);
  nor nor_8 (nor_8_out, and_1_out, nor_6_out);
  nor nor_9 (nor_9_out, STOR, PC_DB_528571a6, D98, D100, T6, T5);
  nor nor_10 (nor_10_out, T0, and_2_out);
  Multiplexer multiplexer_1 (.in0(nor_10_out), .in1(not_8_out), .out(multiplexer_1_out), .sel(L_ready_2ba3d9e7));
  not not_8 (not_8_out, T1);
  nor nor_11 (nor_11_out, not_7_out, NotReadyPhi1);
  D_latch_6baf82dd rdydelay_latch1 (.NOT_Q(rdydelay_latch1_not_q), .D(L_ready_2ba3d9e7), .EN(PHI1));  // open: Q
  nor nor_12 (nor_12_out, and_3_out, nor_7_out);
  D_latch_6baf82dd acr_latch1 (.NOT_Q(acr_latch1_not_q), .D(nor_8_out), .EN(PHI1));  // open: Q
  D_latch_6baf82dd acr_latch2 (.NOT_Q(ACRL2), .D(acr_latch1_not_q), .EN(PHI2));  // open: Q
  D_latch_6baf82dd tresx_latch1 (.Q(tresx_latch1_q), .D(nor_1_out), .EN(PHI2));  // open: NOT_Q
  not not_9 (not_9_out, L_SHIFT_b19c62b1);
  D_latch_6baf82dd wr_latch (.Q(wr_latch_q), .D(nor_9_out), .EN(PHI2));  // open: NOT_Q
  D_latch_6baf82dd ends_latch1 (.Q(ends_latch1_q), .D(multiplexer_1_out), .EN(PHI2));  // open: NOT_Q
  D_latch_6baf82dd ends_latch2 (.Q(ends_latch2_q), .D(RESP), .EN(PHI2));  // open: NOT_Q
  D_latch_6baf82dd nready_latch (.Q(nready_latch_q), .D(not_10_out), .EN(PHI1));  // open: NOT_Q
  not not_10 (not_10_out, L_ready_2ba3d9e7);
  D_latch_6baf82dd br_latch2 (.NOT_Q(br_latch2_not_q), .D(nor_11_out), .EN(PHI2));  // open: Q
  xor xor_1 (xor_1_out, BRFW, not_11_out);
  not not_11 (not_11_out, ACR);
  D_latch_6baf82dd rdydelay_latch2 (.NOT_Q(NotReadyPhi1), .D(rdydelay_latch1_not_q), .EN(PHI2));  // open: Q
  D_latch_6baf82dd comp_latch1 (.Q(comp_latch1_q), .D(TRES1), .EN(PHI1));  // open: NOT_Q
  D_latch_6baf82dd comp_latch2 (.Q(comp_latch2_q), .D(L_TWOCYCLE_43089fae), .EN(PHI1));  // open: NOT_Q
  D_latch_6baf82dd comp_latch3 (.Q(comp_latch3_q), .D(TRESX), .EN(PHI1));  // open: NOT_Q
  D_latch_6baf82dd br_latch1 (.Q(br_latch1_q), .D(nor_12_out), .EN(PHI2));  // open: NOT_Q
  nand nand_1 (nand_1_out, L_SHIFT_b19c62b1, not_1_out);
  nor nor_13 (nor_13_out, D96, not_9_out, L_MemOP_614ba69e);
  and and_4 (and_4_out, comp_latch2_q, comp_latch3_q);
  nor nor_14 (ENDX_Debug, nor_13_out, T6, not_4_out, BR3);
  nor nor_15 (ENDS_Debug, ends_latch1_q, ends_latch2_q);
  and and_5 (and_5_out, ~br_latch2_not_q, xor_1_out);  // AND_Gate
  nor nor_16 (nor_16_out, L_SHIFT_b19c62b1, L_MemOP_614ba69e, L_ready_2ba3d9e7);
  not not_12 (not_12_out, L_ready_2ba3d9e7);
  nor nor_17 (nor_17_out, nor_8_out, tresx_latch1_q, L_ready_2ba3d9e7, nand_1_out);
  nor nor_18 (nor_18_out, comp_latch1_q, and_4_out);
  nor nor_19 (nor_19_out, t0_latch_q, t1x_latch_q);
  and and_6 (and_6_out, t5_latch2_q, L_ready_2ba3d9e7);
  D_latch_6baf82dd t56_latch (.Q(t56_latch_q), .D(nor_16_out), .EN(PHI2));  // open: NOT_Q
  nand nand_2 (nand_2_out, T5, not_12_out);
  nor nor_20 (nor_20_out, L_ready_2ba3d9e7, ENDX_Debug);
  nor nor_21 (nor_21_out, RDY, ready_latch2_q);
  nor nor_22 (WR, L_ready_2ba3d9e7, wr_latch_q, DORES);
  nor nor_23 (nor_23_out, nready_latch_q, RESP, step_latch2_q);
  nor nor_24 (nor_24_out, step_latch1_q, and_5_out);
  nor nor_25 (nor_25_out, nor_24_out, L_ready_2ba3d9e7);
  nor nor_26 (nor_26_out, nor_25_out, ENDS_Debug);
  nor nor_27 (L_T0_be2341f9, nor_18_out, nor_19_out);
  nor nor_28 (nor_28_out, t0_latch_q, L_ready_2ba3d9e7);
  nor nor_29 (nor_29_out, L_ready_2ba3d9e7, br_latch1_q, not_6_out);
  nor nor_30 (nor_30_out, and_6_out, t56_latch_q);
  D_latch_6baf82dd t6_latch1 (.NOT_Q(t6_latch1_not_q), .D(nand_2_out), .EN(PHI2));  // open: Q
  nor nor_31 (TRESX, nor_17_out, BRK6E, tresx_latch2_not_q);
  nor nor_32 (nor_32_out, RESP, ENDS_Debug, nor_20_out);
  D_latch_6baf82dd fetch_latch (.NOT_Q(fetch_latch_not_q), .D(T1), .EN(PHI2));  // open: Q
  D_latch_6baf82dd ready_latch1 (.NOT_Q(ready_latch1_not_q), .D(nor_21_out), .EN(PHI2));  // open: Q
  D_latch_6baf82dd ready_latch2 (.Q(ready_latch2_q), .D(WR), .EN(PHI1));  // open: NOT_Q
  D_latch_6baf82dd step_latch1 (.Q(step_latch1_q), .D(nor_23_out), .EN(PHI2));  // open: NOT_Q
  D_latch_6baf82dd step_latch2 (.Q(step_latch2_q), .D(nor_24_out), .EN(PHI1));  // open: NOT_Q
  D_latch_6baf82dd t1_latch (.NOT_Q(T1), .D(nor_26_out), .EN(PHI1));  // open: Q
  not not_13 (TRES1, nor_26_out);
  D_latch_6baf82dd t0_latch (.Q(t0_latch_q), .D(L_T0_be2341f9), .EN(PHI2));  // open: NOT_Q
  D_latch_6baf82dd t1x_latch (.Q(t1x_latch_q), .NOT_Q(L_T1X_cd47d06e), .D(nor_28_out), .EN(PHI1));
  D_latch_6baf82dd ipc_latch1 (.Q(ipc_latch1_q), .D(B_OUT), .EN(PHI1));  // open: NOT_Q
  D_latch_6baf82dd ipc_latch2 (.Q(ipc_latch2_q), .D(and_5_out), .EN(PHI1));  // open: NOT_Q
  D_latch_6baf82dd ipc_latch3 (.Q(ipc_latch3_q), .D(nor_29_out), .EN(PHI1));  // open: NOT_Q
  D_latch_6baf82dd t5_latch2 (.Q(t5_latch2_q), .D(T5), .EN(PHI2));  // open: NOT_Q
  D_latch_6baf82dd t5_latch1 (.NOT_Q(T5), .D(nor_30_out), .EN(PHI1));  // open: Q
  D_latch_6baf82dd t6_latch2 (.NOT_Q(t6_latch2_not_q), .D(t6_latch1_not_q), .EN(PHI1));  // open: Q
  D_latch_6baf82dd tres2_latch (.NOT_Q(TRES2), .D(TRESX), .EN(PHI1));  // open: Q
  nor nor_33 (STOR, L_MemOP_614ba69e, not_1_out);
  D_latch_6baf82dd tresx_latch2 (.NOT_Q(tresx_latch2_not_q), .D(nor_32_out), .EN(PHI2));  // open: Q
  not not_14 (L_ready_2ba3d9e7, ready_latch1_not_q);
  or or_1 (or_1_out, ipc_latch2_q, ipc_latch3_q);
  not not_15 (T6, t6_latch2_not_q);
  nand nand_3 (L_0_IR_fde7bd13, B_OUT, FETCH);
  nor nor_34 (FETCH, fetch_latch_not_q, L_ready_2ba3d9e7);
  not not_16 (T0, L_T0_be2341f9);
  nand nand_4 (L_1_PC_f7ea2184, ipc_latch1_q, or_1_out);

  // Notes on the sheet:
  //   /STORE
  //   ACRL_FF
  //   STOR
  //   ReadyDelay
  //   TRES1
  //   ACRL1
  //   REST
  //   ENDS
  //   ENDS
  //   RDY
  //   STEP_FF
  //   ENDS
  //   WR
  //   T0_FF
  //   T5_FF
  //   RDY_FF
endmodule

// BUS CONTROL
module BUS_CONTROL (
  input  PHI1,
  input  PHI2,
  input  SBXY,
  input  D55,
  input  D57,
  input  D58,
  input  D59,
  input  D60,
  input  D61,
  input  D62,
  input  D63,
  input  D64,
  input  D65,
  input  D66,
  input  D67,
  input  D68,
  input  AND,
  input  D71,
  input  D72,
  input  D73,
  input  D74,
  input  D79,
  input  STOR,
  input  D81,
  input  D82,
  input  D84,
  input  D89,
  input  D90,
  input  D91,
  input  D83,
  input  D128,
  input  D129,
  input  L_0_ADL0_372ea1ce,
  input  BR2,
  input  ACRL2,
  input  DL_PCH_8d3d82e3,
  input  BR3,
  input  L_ready_2ba3d9e7,
  input  T2,
  input  INC_SB,
  input  D45,
  input  BRK6E,
  input  D46,
  input  D47,
  input  D48,
  input  STXY,
  input  D101,
  input  L_PCH_PCH_45eb8196,
  input  T0,
  input  T1,
  input  T5,
  input  T6,
  input  D56,
  output L_0_ADH0_8d3f04fb,
  output L_0_ADH17_42b6e0bd,
  output SB_AC_692b76aa,
  output ZTST,
  output ADL_ABL_ccbf1bfb,
  output AC_SB_4f3a8e20,
  output SB_DB_92ea0e91,
  output AC_DB_7461a43f,
  output PGX,
  output SB_ADH_3fc727a4,
  output DL_ADH_067137e0,
  output DL_ADL_73e48c13,
  output ADH_ABH_4fac1902,
  output DL_DB_4a6f16a8
);

  wire ac_db_latch_q, ac_sb_latch_q, adh_abh_latch_not_q, adl_abl_latch_not_q, and_1_out, and_2_out,
       and_3_out, and_4_out, and_5_out, and_6_out, dl_adh_latch_not_q, dl_adl_latch_not_q, dl_db_latch_not_q,
       nand_2_out, nand_3_out, nand_4_out, nand_5_out, nor_1_out, nor_2_out, nor_3_out, nor_4_out, nor_5_out,
       nor_6_out, nor_7_out, nor_8_out, nor_9_out, nor_10_out, nor_11_out, nor_12_out, nor_13_out,
       nor_14_out, nor_15_out, nor_16_out, nor_17_out, nor_18_out, nor_19_out, nor_20_out, nor_21_out,
       nor_22_out, nor_23_out, nor_24_out, nor_25_out, not_1_out, not_2_out, not_3_out, not_4_out, not_5_out,
       not_6_out, not_7_out, not_8_out, not_9_out, nready_latch_not_q, or_1_out, sb_ac_latch_q,
       sb_adh_latch_not_q, sb_db_latch_not_q, z_adh17_latch_not_q;

  not not_1 (not_1_out, D64);
  nor nor_1 (nor_1_out, D71, D72);
  not not_2 (not_2_out, D73);
  and and_1 (and_1_out, D79, STOR);
  nor nor_2 (nor_2_out, D81, D82);
  and and_2 (and_2_out, D90, ~D129);  // AND_Gate
  and and_3 (and_3_out, D83, ~D129);  // AND_Gate
  and and_4 (and_4_out, D128, ~D129);  // AND_Gate
  not not_3 (not_3_out, D48);
  nor nor_3 (nor_3_out, D58, D59, D60, D61, D62, D63, D64);
  and and_5 (and_5_out, not_1_out, D65);
  not not_4 (not_4_out, nor_1_out);
  nand nand_1 (PGX, nor_1_out, not_2_out);
  nor nor_4 (nor_4_out, D74, and_1_out);
  nor nor_5 (nor_5_out, D89, and_2_out, D91, D84);
  nor nor_6 (nor_6_out, and_3_out, T0);
  D_latch_6baf82dd nready_latch (.NOT_Q(nready_latch_not_q), .D(L_ready_2ba3d9e7), .EN(PHI1));  // open: Q
  nor nor_7 (nor_7_out, INC_SB, D45, BRK6E, D46, D47, D48);
  nand nand_2 (nand_2_out, not_3_out, STXY);
  not not_5 (not_5_out, nor_3_out);
  nor nor_8 (nor_8_out, and_5_out, AND);
  not not_6 (not_6_out, nor_5_out);
  nor nor_9 (nor_9_out, nor_6_out, and_4_out);
  nand nand_3 (nand_3_out, ACRL2, nready_latch_not_q);
  not not_7 (not_7_out, nor_7_out);
  nand nand_4 (nand_4_out, T5, D55);
  nor nor_10 (nor_10_out, SBXY, not_5_out, T6, AND);
  nor nor_11 (nor_11_out, not_4_out, L_ready_2ba3d9e7);
  nor nor_12 (nor_12_out, PGX, BR3);
  nor nor_13 (nor_13_out, not_6_out, T2, L_PCH_PCH_45eb8196, D56);
  not not_8 (not_8_out, nand_4_out);
  not not_9 (not_9_out, nor_2_out);
  nor nor_14 (nor_14_out, nor_10_out, AND);
  nor nor_15 (nor_15_out, nor_12_out, nand_3_out);
  nor nor_16 (nor_16_out, L_ready_2ba3d9e7, nor_13_out);
  nor nor_17 (nor_17_out, D57, not_9_out);
  or or_1 (or_1_out, nor_15_out, nor_16_out);
  nor nor_18 (nor_18_out, T6, T5);
  nor nor_19 (nor_19_out, not_8_out, nor_14_out, D67, T1, BR2, nand_2_out);
  and and_6 (and_6_out, or_1_out, ~BR3);  // AND_Gate
  nand nand_5 (nand_5_out, nor_18_out, nor_11_out);
  nor nor_20 (nor_20_out, DL_PCH_8d3d82e3, not_6_out);
  nor nor_21 (nor_21_out, L_0_ADL0_372ea1ce, and_6_out);
  nor nor_22 (nor_22_out, BR2, T5);
  D_latch_6baf82dd z_adh0_latch (.NOT_Q(L_0_ADH0_8d3f04fb), .D(nor_2_out), .EN(PHI2));  // open: Q
  D_latch_6baf82dd z_adh17_latch (.NOT_Q(z_adh17_latch_not_q), .D(nor_17_out), .EN(PHI2));  // open: Q
  D_latch_6baf82dd sb_ac_latch (.Q(sb_ac_latch_q), .D(nor_3_out), .EN(PHI2));  // open: NOT_Q
  D_latch_6baf82dd adl_abl_latch (.NOT_Q(adl_abl_latch_not_q), .D(nand_5_out), .EN(PHI2));  // open: Q
  D_latch_6baf82dd ac_sb_latch (.Q(ac_sb_latch_q), .D(nor_8_out), .EN(PHI2));  // open: NOT_Q
  D_latch_6baf82dd sb_db_latch (.NOT_Q(sb_db_latch_not_q), .D(nor_19_out), .EN(PHI2));  // open: Q
  D_latch_6baf82dd ac_db_latch (.Q(ac_db_latch_q), .D(nor_4_out), .EN(PHI2));  // open: NOT_Q
  D_latch_6baf82dd sb_adh_latch (.NOT_Q(sb_adh_latch_not_q), .D(nor_12_out), .EN(PHI2));  // open: Q
  D_latch_6baf82dd dl_adh_latch (.NOT_Q(dl_adh_latch_not_q), .D(nor_20_out), .EN(PHI2));  // open: Q
  D_latch_6baf82dd dl_adl_latch (.NOT_Q(dl_adl_latch_not_q), .D(nor_2_out), .EN(PHI2));  // open: Q
  D_latch_6baf82dd adh_abh_latch (.NOT_Q(adh_abh_latch_not_q), .D(nor_21_out), .EN(PHI2));  // open: Q
  D_latch_6baf82dd dl_db_latch (.NOT_Q(dl_db_latch_not_q), .D(nor_22_out), .EN(PHI2));  // open: Q
  buf buffer_1 (L_0_ADH17_42b6e0bd, z_adh17_latch_not_q);
  buf buffer_2 (SB_AC_692b76aa, nor_23_out);
  nor nor_23 (nor_23_out, sb_ac_latch_q, PHI2);
  not not_10 (ZTST, nor_10_out);
  buf buffer_3 (ADL_ABL_ccbf1bfb, adl_abl_latch_not_q);
  buf buffer_4 (AC_SB_4f3a8e20, nor_24_out);
  nor nor_24 (nor_24_out, ac_sb_latch_q, PHI2);
  buf buffer_5 (SB_DB_92ea0e91, sb_db_latch_not_q);
  buf buffer_6 (AC_DB_7461a43f, nor_25_out);
  nor nor_25 (nor_25_out, ac_db_latch_q, PHI2);
  buf buffer_7 (SB_ADH_3fc727a4, sb_adh_latch_not_q);
  buf buffer_8 (DL_ADH_067137e0, dl_adh_latch_not_q);
  buf buffer_9 (DL_ADL_73e48c13, dl_adl_latch_not_q);
  buf buffer_10 (ADH_ABH_4fac1902, adh_abh_latch_not_q);
  buf buffer_11 (DL_DB_4a6f16a8, dl_db_latch_not_q);

  // Other names for the same wires on the sheet: RTS_5_f937778f = D84

  // Notes on the sheet:
  //   BR0
  //   STA
  //   push/pull
  //   JSR2
  //   #DL/ADL
  //   ABS/2
  //   #SB/AC
  //   PGX
  //   IMPLIED
  //   JSR/5
  //   SBXY
  //   AND
  //   IND
  //   #DL/ADL
  //   #ZTST
  //   SBA
  //   JSXY
  //   JSXY
  //   JMP/4
  //   #DL/ADL
  //   #SB/AC
  //   #ADL/ABL
  //   #AC/SB
  //   #SB/DB
  //   #DL/ADL
  //   #DL/DB
endmodule

// FLAGS CONTROL
module FLAGS_CONTROL (
  input  PHI2,
  input  D98,
  input  D99,
  input  D108,
  input  D110,
  input  D120,
  input  D127,
  input  D107,
  input  T6,
  input  D112,
  input  D116,
  input  D117,
  input  D118,
  input  D119,
  input  ZTST,
  input  D109,
  input  L_ready_2ba3d9e7,
  input  SR,
  input  D114,
  input  D115,
  input  D113,
  output P_DB_0ea80532,
  output IR5_I_a8b17eb4,
  output IR5_C_bb157132,
  output IR5_D_a37efeb0,
  output L_0_V_6d5b0af2,
  output ACR_C_fc5559e8,
  output DBZ_Z_805d2a94,
  output DB_N_4f1ad326,
  output DB_P_0fe10735,
  output DB_C_acfbba71,
  output DB_V_9eaeb3a2
);

  wire and_1_out, and_2_out, bit_latch_q, dbn_latch_q, dbz_latch_q, nor_1_out, nor_2_out, nor_3_out,
       nor_4_out, nor_5_out, not_1_out, not_2_out, not_3_out, not_4_out, not_5_out, pin_latch_q;

  nor nor_1 (nor_1_out, D98, D99);
  not not_1 (not_1_out, D108);
  not not_2 (not_2_out, D110);
  not not_3 (not_3_out, D120);
  not not_4 (not_4_out, D127);
  and and_1 (and_1_out, D107, T6);
  nor nor_2 (nor_2_out, D114, D115);
  not not_5 (not_5_out, D113);
  nor nor_3 (nor_3_out, and_1_out, D112, D116, D117, D118, D119);
  nor nor_4 (nor_4_out, ACR_C_fc5559e8, ZTST, D109);
  nor nor_5 (nor_5_out, SR, DB_P_0fe10735);
  D_latch_6baf82dd pdb_latch (.NOT_Q(P_DB_0ea80532), .D(nor_1_out), .EN(PHI2));  // open: Q
  D_latch_6baf82dd iri_latch (.NOT_Q(IR5_I_a8b17eb4), .D(not_1_out), .EN(PHI2));  // open: Q
  D_latch_6baf82dd irc_latch (.NOT_Q(IR5_C_bb157132), .D(not_2_out), .EN(PHI2));  // open: Q
  D_latch_6baf82dd ird_latch (.NOT_Q(IR5_D_a37efeb0), .D(not_3_out), .EN(PHI2));  // open: Q
  D_latch_6baf82dd zv_latch (.NOT_Q(L_0_V_6d5b0af2), .D(not_4_out), .EN(PHI2));  // open: Q
  D_latch_6baf82dd acrc_latch (.NOT_Q(ACR_C_fc5559e8), .D(nor_3_out), .EN(PHI2));  // open: Q
  D_latch_6baf82dd dbz_latch (.Q(dbz_latch_q), .NOT_Q(DBZ_Z_805d2a94), .D(nor_4_out), .EN(PHI2));
  D_latch_6baf82dd dbn_latch (.Q(dbn_latch_q), .D(D109), .EN(PHI2));  // open: NOT_Q
  D_latch_6baf82dd dbc_latch (.NOT_Q(DB_C_acfbba71), .D(nor_5_out), .EN(PHI2));  // open: Q
  D_latch_6baf82dd pin_latch (.Q(pin_latch_q), .D(nor_2_out), .EN(PHI2));  // open: NOT_Q
  D_latch_6baf82dd bit_latch (.Q(bit_latch_q), .D(not_5_out), .EN(PHI2));  // open: NOT_Q
  and and_2 (and_2_out, dbz_latch_q, pin_latch_q);
  nor nor_6 (DB_P_0fe10735, pin_latch_q, L_ready_2ba3d9e7);
  nand nand_1 (DB_V_9eaeb3a2, pin_latch_q, bit_latch_q);
  nor nor_7 (DB_N_4f1ad326, and_2_out, dbn_latch_q);

  // Notes on the sheet:
  //   AVR/V
  //   BIT1
  //   BIT0
  //   /POUT
  //   /CSI
  //   ZTST
  //   /PIN
  //   /ARIT
  //   BIT1
endmodule

module FLAGS (
  input  P_DB_0ea80532,
  input  B_OUT,
  input  in_3,
  input  in_4,
  input  in_5,
  input  in_6,
  input  DB4,
  input  DB5,
  input  in_9,
  input  in_10,
  input  DB_P_0fe10735,
  input  DBZ_Z_805d2a94,
  input  DB_N_4f1ad326,
  input  IR5_C_bb157132,
  input  ACR,
  input  DB_C_acfbba71,
  input  ACR_C_fc5559e8,
  input  IR5_D_a37efeb0,
  input  PHI1,
  input  PHI2,
  input  L_IR5_7bf6fd52,
  input  IR5_I_a8b17eb4,
  input  BRK6E,
  input  AVR,
  input  DB_V_9eaeb3a2,
  input  D112,
  input  L_0_V_6d5b0af2,
  input  SO,
  output DB0,
  output DB1,
  output DB2,
  output DB3,
  output out_33,
  output N_C,
  output DB6,
  output DB7,
  output L_Z_OUT_273329d7,
  output L_N_OUT_f0a30453,
  output L_C_OUT_e01a0d59,
  output L_D_OUT_eaa1b777,
  output L_I_OUT_a88ea15a,
  output L_V_OUT_cf6c2405
);

  wire and_1_out, and_2_out, and_3_out, and_4_out, and_5_out, and_6_out, and_7_out, and_8_out, and_9_out,
       and_10_out, and_11_out, and_12_out, and_13_out, and_14_out, and_15_out, and_16_out, and_17_out,
       and_18_out, avr_latch_q, c_latch2_q, d_latch2_q, i_latch1_not_q, i_latch2_q, n_latch2_q, nor_1_out,
       nor_2_out, nor_3_out, nor_4_out, nor_5_out, nor_6_out, nor_7_out, nor_8_out, nor_9_out, nor_10_out,
       nor_11_out, nor_12_out, nor_13_out, not_1_out, not_2_out, not_3_out, not_4_out, not_5_out, not_6_out,
       not_7_out, not_8_out, not_9_out, not_10_out, not_11_out, not_12_out, not_13_out, not_14_out,
       not_15_out, not_16_out, not_17_out, so_latch1_not_q, so_latch2_not_q, so_latch3_q, v_latch2_q,
       vset_latch_q, z_latch2_q;

  D_latch_6baf82dd avr_latch (.Q(avr_latch_q), .D(D112), .EN(PHI2));  // open: NOT_Q
  not not_1 (not_1_out, SO);
  nor nor_1 (nor_1_out, in_3, in_4, in_5, in_6, DB4, DB5, in_9, in_10);
  not not_2 (not_2_out, in_4);
  not not_3 (not_3_out, nor_1_out);
  not not_4 (not_4_out, in_10);
  nor nor_2 (nor_2_out, DB_P_0fe10735, DBZ_Z_805d2a94);
  not not_5 (not_5_out, DB_N_4f1ad326);
  not not_6 (not_6_out, ACR);
  not not_7 (not_7_out, in_3);
  nor nor_3 (nor_3_out, DB_C_acfbba71, IR5_C_bb157132, ACR_C_fc5559e8);
  not not_8 (not_8_out, in_6);
  nor nor_4 (nor_4_out, IR5_D_a37efeb0, DB_P_0fe10735);
  not not_9 (not_9_out, in_5);
  nor nor_5 (nor_5_out, DB_P_0fe10735, IR5_I_a8b17eb4);
  not not_10 (not_10_out, AVR);
  not not_11 (not_11_out, in_9);
  nor nor_6 (nor_6_out, DB_V_9eaeb3a2, avr_latch_q, vset_latch_q);
  D_latch_6baf82dd so_latch1 (.NOT_Q(so_latch1_not_q), .D(not_1_out), .EN(PHI1));  // open: Q
  and and_1 (and_1_out, not_2_out, DB_P_0fe10735);
  and and_2 (and_2_out, not_3_out, DBZ_Z_805d2a94);
  and and_3 (and_3_out, nor_2_out, z_latch2_q);
  and and_4 (and_4_out, not_4_out, DB_N_4f1ad326);
  and and_5 (and_5_out, not_5_out, n_latch2_q);
  and and_6 (and_6_out, L_IR5_7bf6fd52, IR5_C_bb157132);
  and and_7 (and_7_out, not_6_out, ACR_C_fc5559e8);
  and and_8 (and_8_out, not_7_out, DB_C_acfbba71);
  and and_9 (and_9_out, nor_3_out, c_latch2_q);
  and and_10 (and_10_out, IR5_D_a37efeb0, L_IR5_7bf6fd52);
  and and_11 (and_11_out, not_8_out, DB_P_0fe10735);
  and and_12 (and_12_out, nor_4_out, d_latch2_q);
  and and_13 (and_13_out, L_IR5_7bf6fd52, IR5_I_a8b17eb4);
  and and_14 (and_14_out, not_9_out, DB_P_0fe10735);
  and and_15 (and_15_out, nor_5_out, i_latch2_q);
  and and_16 (and_16_out, not_10_out, avr_latch_q);
  and and_17 (and_17_out, not_11_out, DB_V_9eaeb3a2);
  and and_18 (and_18_out, nor_6_out, v_latch2_q);
  D_latch_6baf82dd so_latch2 (.NOT_Q(so_latch2_not_q), .D(so_latch1_not_q), .EN(PHI2));  // open: Q
  nor nor_7 (nor_7_out, and_1_out, and_2_out, and_3_out);
  nor nor_8 (nor_8_out, and_4_out, and_5_out);
  nor nor_9 (nor_9_out, and_6_out, and_7_out, and_8_out, and_9_out);
  nor nor_10 (nor_10_out, and_10_out, and_11_out, and_12_out);
  nor nor_11 (nor_11_out, and_13_out, and_14_out, and_15_out);
  nor nor_12 (nor_12_out, and_16_out, and_17_out, and_18_out, L_0_V_6d5b0af2);
  D_latch_6baf82dd so_latch3 (.Q(so_latch3_q), .D(so_latch2_not_q), .EN(PHI1));  // open: NOT_Q
  nor nor_13 (nor_13_out, so_latch3_q, so_latch1_not_q);
  D_latch_6baf82dd z_latch1 (.NOT_Q(L_Z_OUT_273329d7), .D(nor_7_out), .EN(PHI1));  // open: Q
  D_latch_6baf82dd z_latch2 (.Q(z_latch2_q), .D(L_Z_OUT_273329d7), .EN(PHI2));  // open: NOT_Q
  D_latch_6baf82dd n_latch1 (.NOT_Q(L_N_OUT_f0a30453), .D(nor_8_out), .EN(PHI1));  // open: Q
  D_latch_6baf82dd n_latch2 (.Q(n_latch2_q), .D(L_N_OUT_f0a30453), .EN(PHI2));  // open: NOT_Q
  D_latch_6baf82dd c_latch1 (.NOT_Q(L_C_OUT_e01a0d59), .D(nor_9_out), .EN(PHI1));  // open: Q
  D_latch_6baf82dd c_latch2 (.Q(c_latch2_q), .D(L_C_OUT_e01a0d59), .EN(PHI2));  // open: NOT_Q
  D_latch_6baf82dd d_latch1 (.NOT_Q(L_D_OUT_eaa1b777), .D(nor_10_out), .EN(PHI1));  // open: Q
  D_latch_6baf82dd d_latch2 (.Q(d_latch2_q), .D(L_D_OUT_eaa1b777), .EN(PHI2));  // open: NOT_Q
  D_latch_6baf82dd i_latch1 (.NOT_Q(i_latch1_not_q), .D(nor_11_out), .EN(PHI1));  // open: Q
  D_latch_6baf82dd i_latch2 (.Q(i_latch2_q), .D(L_I_OUT_a88ea15a), .EN(PHI2));  // open: NOT_Q
  D_latch_6baf82dd v_latch1 (.NOT_Q(L_V_OUT_cf6c2405), .D(nor_12_out), .EN(PHI1));  // open: Q
  D_latch_6baf82dd v_latch2 (.Q(v_latch2_q), .D(L_V_OUT_cf6c2405), .EN(PHI2));  // open: NOT_Q
  D_latch_6baf82dd vset_latch (.Q(vset_latch_q), .D(nor_13_out), .EN(PHI2));  // open: NOT_Q
  and and_19 (L_I_OUT_a88ea15a, ~BRK6E, i_latch1_not_q);  // AND_Gate
  assign DB0 = P_DB_0ea80532 ? not_12_out : 1'bz;  // Controlled_Buffer controlled_buffer_1
  not not_12 (not_12_out, L_C_OUT_e01a0d59);
  assign DB1 = P_DB_0ea80532 ? not_13_out : 1'bz;  // Controlled_Buffer controlled_buffer_2
  not not_13 (not_13_out, L_Z_OUT_273329d7);
  assign DB2 = P_DB_0ea80532 ? not_14_out : 1'bz;  // Controlled_Buffer controlled_buffer_3
  not not_14 (not_14_out, L_I_OUT_a88ea15a);
  assign DB3 = P_DB_0ea80532 ? not_15_out : 1'bz;  // Controlled_Buffer controlled_buffer_4
  not not_15 (not_15_out, L_D_OUT_eaa1b777);
  assign out_33 = P_DB_0ea80532 ? B_OUT : 1'bz;  // Controlled_Buffer controlled_buffer_5
  assign DB6 = P_DB_0ea80532 ? not_16_out : 1'bz;  // Controlled_Buffer controlled_buffer_6
  not not_16 (not_16_out, L_V_OUT_cf6c2405);
  assign DB7 = P_DB_0ea80532 ? not_17_out : 1'bz;  // Controlled_Buffer controlled_buffer_7
  not not_17 (not_17_out, L_N_OUT_f0a30453);

  // Other names for the same wires on the sheet: DB0_t = in_3; DB2_t = in_5; DB3_t = in_6; DB6_t = in_9

  // Notes on the sheet:
  //   AVR/V
  //   ACR/C
  //   /DB1
  //   /DBZ
  //   /DB7
  //   DB/C
  //   IR5/D
  //   IR5/I
  //   DB/V
  //   1/V
  //   IR5/C
  //   /ACR
  //   ACR/C
  //   /DB0
  //   DB/C
  //   IR5/D
  //   /DB3
  //   IR5/I
  //   /DB2
  //   /AVR
  //   /DB6
  //   DB/V
  //   0/V
  //   Z FLAG
  //   /Z_OUT
  //   N FLAG
  //   /N_OUT
  //   C FLAG
  //   /C_OUT
  //   D FLAG
  //   /D_OUT
  //   I FLAG
  //   V FLAG
  //   /V_OUT
  //   /I_OUT
endmodule

module ABH (
  input  PHI1,
  input  PHI2,
  input  ADH_ABH_4fac1902,
  input  ADH0,
  input  ADH1,
  input  ADH2,
  input  ADH3,
  input  ADH4,
  input  ADH5,
  input  ADH6,
  input  ADH7,
  output A8,
  output A9,
  output A10,
  output A11,
  output A12,
  output A13,
  output A14,
  output A15
);

  ABH_BIT _0 (.Ax(A8), .ADH_ABH_4fac1902(ADH_ABH_4fac1902), .ADHx(ADH0), .PHI1(PHI1), .PHI2(PHI2));
  ABH_BIT _1 (.Ax(A9), .ADH_ABH_4fac1902(ADH_ABH_4fac1902), .ADHx(ADH1), .PHI1(PHI1), .PHI2(PHI2));
  ABH_BIT _2 (.Ax(A10), .ADH_ABH_4fac1902(ADH_ABH_4fac1902), .ADHx(ADH2), .PHI1(PHI1), .PHI2(PHI2));
  ABH_BIT _3 (.Ax(A11), .ADH_ABH_4fac1902(ADH_ABH_4fac1902), .ADHx(ADH3), .PHI1(PHI1), .PHI2(PHI2));
  ABH_BIT _4 (.Ax(A12), .ADH_ABH_4fac1902(ADH_ABH_4fac1902), .ADHx(ADH4), .PHI1(PHI1), .PHI2(PHI2));
  ABH_BIT _5 (.Ax(A13), .ADH_ABH_4fac1902(ADH_ABH_4fac1902), .ADHx(ADH5), .PHI1(PHI1), .PHI2(PHI2));
  ABH_BIT _6 (.Ax(A14), .ADH_ABH_4fac1902(ADH_ABH_4fac1902), .ADHx(ADH6), .PHI1(PHI1), .PHI2(PHI2));
  ABH_BIT _7 (.Ax(A15), .ADH_ABH_4fac1902(ADH_ABH_4fac1902), .ADHx(ADH7), .PHI1(PHI1), .PHI2(PHI2));
endmodule

module ABL (
  input  PHI1,
  input  PHI2,
  input  ADL_ABL_ccbf1bfb,
  input  ADL0,
  input  ADL1,
  input  ADL2,
  input  ADL3,
  input  ADL4,
  input  ADL5,
  input  ADL6,
  input  ADL7,
  output A0,
  output A1,
  output A2,
  output A3,
  output A4,
  output A5,
  output A6,
  output A7
);

  ABL_BIT _0 (.Ax(A0), .ADL_ABL_ccbf1bfb(ADL_ABL_ccbf1bfb), .ADLx(ADL0), .PHI1(PHI1), .PHI2(PHI2));
  ABL_BIT _1 (.Ax(A1), .ADL_ABL_ccbf1bfb(ADL_ABL_ccbf1bfb), .ADLx(ADL1), .PHI1(PHI1), .PHI2(PHI2));
  ABL_BIT _2 (.Ax(A2), .ADL_ABL_ccbf1bfb(ADL_ABL_ccbf1bfb), .ADLx(ADL2), .PHI1(PHI1), .PHI2(PHI2));
  ABL_BIT _3 (.Ax(A3), .ADL_ABL_ccbf1bfb(ADL_ABL_ccbf1bfb), .ADLx(ADL3), .PHI1(PHI1), .PHI2(PHI2));
  ABL_BIT _4 (.Ax(A4), .ADL_ABL_ccbf1bfb(ADL_ABL_ccbf1bfb), .ADLx(ADL4), .PHI1(PHI1), .PHI2(PHI2));
  ABL_BIT _5 (.Ax(A5), .ADL_ABL_ccbf1bfb(ADL_ABL_ccbf1bfb), .ADLx(ADL5), .PHI1(PHI1), .PHI2(PHI2));
  ABL_BIT _6 (.Ax(A6), .ADL_ABL_ccbf1bfb(ADL_ABL_ccbf1bfb), .ADLx(ADL6), .PHI1(PHI1), .PHI2(PHI2));
  ABL_BIT _7 (.Ax(A7), .ADL_ABL_ccbf1bfb(ADL_ABL_ccbf1bfb), .ADLx(ADL7), .PHI1(PHI1), .PHI2(PHI2));
endmodule

module REGS_BIT (
  input  PHI2,
  input  Y_SB_981fc62c,
  input  SB_Y_f952d371,
  input  X_SB_50e8fb84,
  input  SB_X_a4a389b1,
  input  S_ADL_299349f9,
  input  S_S_0e77937e,
  input  SB_S_e7e7b943,
  input  S_SB_c8f0deaa,
  input  SBx_In,
  output SBx,
  output ADLx,
  output Y_Debug,
  output X_Debug,
  output S_Debug
);

  wire and_1_out, and_2_out, multiplexer_1_out, not_1_out, not_2_out, not_3_out, S_in_not_q;

  not not_1 (not_1_out, PHI2);
  not not_2 (not_2_out, PHI2);
  not not_3 (not_3_out, PHI2);
  Multiplexer #(.enable("true")) multiplexer_1 (
    .in0(S_Debug), .in1(SBx_In), .out(multiplexer_1_out), .sel(SB_S_e7e7b943));  // open: en
  D_Flip_Flop #(.trigger("high")) Y (.D(SBx_In), .clk(and_1_out), .Q(Y_Debug));  // open: Qn, preset, reset
  and and_1 (and_1_out, not_1_out, SB_Y_f952d371);
  D_Flip_Flop #(.trigger("high")) X (.D(SBx_In), .clk(and_2_out), .Q(X_Debug));  // open: Qn, preset, reset
  and and_2 (and_2_out, not_2_out, SB_X_a4a389b1);
  D_latch_6baf82dd S_in (.NOT_Q(S_in_not_q), .D(multiplexer_1_out), .EN(not_3_out));  // open: Q
  D_latch_6baf82dd S_out (.NOT_Q(S_Debug), .D(S_in_not_q), .EN(PHI2));  // open: Q
  assign SBx = Y_SB_981fc62c ? Y_Debug : 1'bz;  // Controlled_Buffer controlled_buffer_1
  assign SBx = X_SB_50e8fb84 ? X_Debug : 1'bz;  // Controlled_Buffer controlled_buffer_2
  assign SBx = S_SB_c8f0deaa ? S_Debug : 1'bz;  // Controlled_Buffer controlled_buffer_3
  assign ADLx = S_ADL_299349f9 ? S_Debug : 1'bz;  // Controlled_Buffer controlled_buffer_4

  // Notes on the sheet:
  //   unused
endmodule

module REGS (
  input  PHI2,
  input  Y_SB_981fc62c,
  input  SB_Y_f952d371,
  input  X_SB_50e8fb84,
  input  SB_X_a4a389b1,
  input  S_ADL_299349f9,
  input  S_S_0e77937e,
  input  SB_S_e7e7b943,
  input  S_SB_c8f0deaa,
  input  SB0,
  input  SB1,
  input  SB2,
  input  in_13,
  input  in_14,
  input  in_15,
  input  SB6,
  input  SB7,
  output out_18,
  output out_19,
  output out_20,
  output SB3,
  output SB4,
  output SB5,
  output out_24,
  output out_25,
  output ADL0,
  output ADL1,
  output ADL2,
  output ADL3,
  output ADL4,
  output ADL5,
  output ADL6,
  output ADL7,
  output [7:0] S_Debug,
  output [7:0] Y_Debug,
  output [7:0] X_Debug
);

  REGS_BIT _0 (
    .ADLx(ADL0), .Y_Debug(Y_Debug[0]), .X_Debug(X_Debug[0]), .S_Debug(S_Debug[0]), .SBx(out_18),
    .Y_SB_981fc62c(Y_SB_981fc62c), .SB_Y_f952d371(SB_Y_f952d371), .X_SB_50e8fb84(X_SB_50e8fb84),
    .SB_X_a4a389b1(SB_X_a4a389b1), .S_ADL_299349f9(S_ADL_299349f9), .S_S_0e77937e(S_S_0e77937e),
    .SB_S_e7e7b943(SB_S_e7e7b943), .S_SB_c8f0deaa(S_SB_c8f0deaa), .SBx_In(SB0), .PHI2(PHI2));
  REGS_BIT _4 (
    .ADLx(ADL4), .Y_Debug(Y_Debug[4]), .X_Debug(X_Debug[4]), .S_Debug(S_Debug[4]), .SBx(SB4),
    .Y_SB_981fc62c(Y_SB_981fc62c), .SB_Y_f952d371(SB_Y_f952d371), .X_SB_50e8fb84(X_SB_50e8fb84),
    .SB_X_a4a389b1(SB_X_a4a389b1), .S_ADL_299349f9(S_ADL_299349f9), .S_S_0e77937e(S_S_0e77937e),
    .SB_S_e7e7b943(SB_S_e7e7b943), .S_SB_c8f0deaa(S_SB_c8f0deaa), .SBx_In(in_14), .PHI2(PHI2));
  REGS_BIT _1 (
    .ADLx(ADL1), .Y_Debug(Y_Debug[1]), .X_Debug(X_Debug[1]), .S_Debug(S_Debug[1]), .SBx(out_19),
    .Y_SB_981fc62c(Y_SB_981fc62c), .SB_Y_f952d371(SB_Y_f952d371), .X_SB_50e8fb84(X_SB_50e8fb84),
    .SB_X_a4a389b1(SB_X_a4a389b1), .S_ADL_299349f9(S_ADL_299349f9), .S_S_0e77937e(S_S_0e77937e),
    .SB_S_e7e7b943(SB_S_e7e7b943), .S_SB_c8f0deaa(S_SB_c8f0deaa), .SBx_In(SB1), .PHI2(PHI2));
  REGS_BIT _5 (
    .ADLx(ADL5), .Y_Debug(Y_Debug[5]), .X_Debug(X_Debug[5]), .S_Debug(S_Debug[5]), .SBx(SB5),
    .Y_SB_981fc62c(Y_SB_981fc62c), .SB_Y_f952d371(SB_Y_f952d371), .X_SB_50e8fb84(X_SB_50e8fb84),
    .SB_X_a4a389b1(SB_X_a4a389b1), .S_ADL_299349f9(S_ADL_299349f9), .S_S_0e77937e(S_S_0e77937e),
    .SB_S_e7e7b943(SB_S_e7e7b943), .S_SB_c8f0deaa(S_SB_c8f0deaa), .SBx_In(in_15), .PHI2(PHI2));
  REGS_BIT _2 (
    .ADLx(ADL2), .Y_Debug(Y_Debug[2]), .X_Debug(X_Debug[2]), .S_Debug(S_Debug[2]), .SBx(out_20),
    .Y_SB_981fc62c(Y_SB_981fc62c), .SB_Y_f952d371(SB_Y_f952d371), .X_SB_50e8fb84(X_SB_50e8fb84),
    .SB_X_a4a389b1(SB_X_a4a389b1), .S_ADL_299349f9(S_ADL_299349f9), .S_S_0e77937e(S_S_0e77937e),
    .SB_S_e7e7b943(SB_S_e7e7b943), .S_SB_c8f0deaa(S_SB_c8f0deaa), .SBx_In(SB2), .PHI2(PHI2));
  REGS_BIT _6 (
    .ADLx(ADL6), .Y_Debug(Y_Debug[6]), .X_Debug(X_Debug[6]), .S_Debug(S_Debug[6]), .SBx(out_24),
    .Y_SB_981fc62c(Y_SB_981fc62c), .SB_Y_f952d371(SB_Y_f952d371), .X_SB_50e8fb84(X_SB_50e8fb84),
    .SB_X_a4a389b1(SB_X_a4a389b1), .S_ADL_299349f9(S_ADL_299349f9), .S_S_0e77937e(S_S_0e77937e),
    .SB_S_e7e7b943(SB_S_e7e7b943), .S_SB_c8f0deaa(S_SB_c8f0deaa), .SBx_In(SB6), .PHI2(PHI2));
  REGS_BIT _3 (
    .ADLx(ADL3), .Y_Debug(Y_Debug[3]), .X_Debug(X_Debug[3]), .S_Debug(S_Debug[3]), .SBx(SB3),
    .Y_SB_981fc62c(Y_SB_981fc62c), .SB_Y_f952d371(SB_Y_f952d371), .X_SB_50e8fb84(X_SB_50e8fb84),
    .SB_X_a4a389b1(SB_X_a4a389b1), .S_ADL_299349f9(S_ADL_299349f9), .S_S_0e77937e(S_S_0e77937e),
    .SB_S_e7e7b943(SB_S_e7e7b943), .S_SB_c8f0deaa(S_SB_c8f0deaa), .SBx_In(in_13), .PHI2(PHI2));
  REGS_BIT _7 (
    .ADLx(ADL7), .Y_Debug(Y_Debug[7]), .X_Debug(X_Debug[7]), .S_Debug(S_Debug[7]), .SBx(out_25),
    .Y_SB_981fc62c(Y_SB_981fc62c), .SB_Y_f952d371(SB_Y_f952d371), .X_SB_50e8fb84(X_SB_50e8fb84),
    .SB_X_a4a389b1(SB_X_a4a389b1), .S_ADL_299349f9(S_ADL_299349f9), .S_S_0e77937e(S_S_0e77937e),
    .SB_S_e7e7b943(SB_S_e7e7b943), .S_SB_c8f0deaa(S_SB_c8f0deaa), .SBx_In(SB7), .PHI2(PHI2));
endmodule

module DL_BIT (
  input  PHI1,
  input  PHI2,
  input  DL_ADL_73e48c13,
  input  DL_ADH_067137e0,
  input  DL_DB_4a6f16a8,
  input  RD,
  input  DBx,
  input  Dx,
  output ADLx,
  output ADHx,
  output out_11,
  output out_12,
  output DOR_Debug,
  output DL_Debug
);

  wire and_1_out, and_2_out, and_3_out, not_1_out, not_2_out, not_3_out;

  D_latch_6baf82dd DL (.NOT_Q(DL_Debug), .D(not_1_out), .EN(PHI2));  // open: Q
  not not_1 (not_1_out, Dx);
  D_latch_6baf82dd DOR (.NOT_Q(DOR_Debug), .D(not_2_out), .EN(PHI1));  // open: Q
  not not_2 (not_2_out, DBx);
  and and_1 (and_1_out, DL_ADL_73e48c13, PHI1);
  and and_2 (and_2_out, DL_ADH_067137e0, PHI1);
  and and_3 (and_3_out, DL_DB_4a6f16a8, PHI1);
  not not_3 (not_3_out, RD);
  assign ADLx = and_1_out ? DL_Debug : 1'bz;  // Controlled_Buffer controlled_buffer_1
  assign ADHx = and_2_out ? DL_Debug : 1'bz;  // Controlled_Buffer controlled_buffer_2
  assign out_11 = and_3_out ? DL_Debug : 1'bz;  // Controlled_Buffer controlled_buffer_3
  assign out_12 = not_3_out ? DOR_Debug : 1'bz;  // Controlled_Buffer controlled_buffer_4
endmodule

module DL (
  input  PHI1,
  input  PHI2,
  input  WR,
  input  DL_ADL_73e48c13,
  input  DL_ADH_067137e0,
  input  DL_DB_4a6f16a8,
  input  in_7,
  input  in_8,
  input  in_9,
  input  in_10,
  input  DB4,
  input  in_12,
  input  DB6,
  input  in_14,
  input  D0,
  input  D1,
  input  D2,
  input  D3,
  input  D4,
  input  in_20,
  input  D6,
  input  in_22,
  output DB0,
  output DB1,
  output DB2,
  output DB3,
  output out_27,
  output DB5,
  output out_29,
  output DB7,
  output ADL0,
  output ADL1,
  output ADL2,
  output ADL3,
  output ADL4,
  output ADL5,
  output ADL6,
  output ADL7,
  output ADH0,
  output ADH1,
  output ADH2,
  output ADH3,
  output ADH4,
  output ADH5,
  output ADH6,
  output ADH7,
  output out_47,
  output out_48,
  output out_49,
  output out_50,
  output out_51,
  output D5,
  output out_53,
  output D7,
  output [7:0] DL_Debug,
  output [7:0] DOR_Debug
);

  wire d_latch_6baf82dd_1_not_q, RD;

  D_latch_6baf82dd d_latch_6baf82dd_1 (.NOT_Q(d_latch_6baf82dd_1_not_q), .D(WR), .EN(PHI1));  // open: Q
  Multiplexer multiplexer_1 (.in0(d_latch_6baf82dd_1_not_q), .in1(1'b1), .out(RD), .sel(PHI2));
  DL_BIT _0 (
    .ADLx(ADL0), .ADHx(ADH0), .out_11(DB0), .out_12(out_47), .DOR_Debug(DOR_Debug[0]),
    .DL_Debug(DL_Debug[0]), .DL_ADL_73e48c13(DL_ADL_73e48c13), .DL_ADH_067137e0(DL_ADH_067137e0),
    .DL_DB_4a6f16a8(DL_DB_4a6f16a8), .RD(RD), .DBx(in_7), .Dx(D0), .PHI1(PHI1), .PHI2(PHI2));
  DL_BIT _1 (
    .ADLx(ADL1), .ADHx(ADH1), .out_11(DB1), .out_12(out_48), .DOR_Debug(DOR_Debug[1]),
    .DL_Debug(DL_Debug[1]), .DL_ADL_73e48c13(DL_ADL_73e48c13), .DL_ADH_067137e0(DL_ADH_067137e0),
    .DL_DB_4a6f16a8(DL_DB_4a6f16a8), .RD(RD), .DBx(in_8), .Dx(D1), .PHI1(PHI1), .PHI2(PHI2));
  DL_BIT _2 (
    .ADLx(ADL2), .ADHx(ADH2), .out_11(DB2), .out_12(out_49), .DOR_Debug(DOR_Debug[2]),
    .DL_Debug(DL_Debug[2]), .DL_ADL_73e48c13(DL_ADL_73e48c13), .DL_ADH_067137e0(DL_ADH_067137e0),
    .DL_DB_4a6f16a8(DL_DB_4a6f16a8), .RD(RD), .DBx(in_9), .Dx(D2), .PHI1(PHI1), .PHI2(PHI2));
  DL_BIT _3 (
    .ADLx(ADL3), .ADHx(ADH3), .out_11(DB3), .out_12(out_50), .DOR_Debug(DOR_Debug[3]),
    .DL_Debug(DL_Debug[3]), .DL_ADL_73e48c13(DL_ADL_73e48c13), .DL_ADH_067137e0(DL_ADH_067137e0),
    .DL_DB_4a6f16a8(DL_DB_4a6f16a8), .RD(RD), .DBx(in_10), .Dx(D3), .PHI1(PHI1), .PHI2(PHI2));
  DL_BIT _4 (
    .ADLx(ADL4), .ADHx(ADH4), .out_11(out_27), .out_12(out_51), .DOR_Debug(DOR_Debug[4]),
    .DL_Debug(DL_Debug[4]), .DL_ADL_73e48c13(DL_ADL_73e48c13), .DL_ADH_067137e0(DL_ADH_067137e0),
    .DL_DB_4a6f16a8(DL_DB_4a6f16a8), .RD(RD), .DBx(DB4), .Dx(D4), .PHI1(PHI1), .PHI2(PHI2));
  DL_BIT _5 (
    .ADLx(ADL5), .ADHx(ADH5), .out_11(DB5), .out_12(D5), .DOR_Debug(DOR_Debug[5]), .DL_Debug(DL_Debug[5]),
    .DL_ADL_73e48c13(DL_ADL_73e48c13), .DL_ADH_067137e0(DL_ADH_067137e0), .DL_DB_4a6f16a8(DL_DB_4a6f16a8),
    .RD(RD), .DBx(in_12), .Dx(in_20), .PHI1(PHI1), .PHI2(PHI2));
  DL_BIT _6 (
    .ADLx(ADL6), .ADHx(ADH6), .out_11(out_29), .out_12(out_53), .DOR_Debug(DOR_Debug[6]),
    .DL_Debug(DL_Debug[6]), .DL_ADL_73e48c13(DL_ADL_73e48c13), .DL_ADH_067137e0(DL_ADH_067137e0),
    .DL_DB_4a6f16a8(DL_DB_4a6f16a8), .RD(RD), .DBx(DB6), .Dx(D6), .PHI1(PHI1), .PHI2(PHI2));
  DL_BIT _7 (
    .ADLx(ADL7), .ADHx(ADH7), .out_11(DB7), .out_12(D7), .DOR_Debug(DOR_Debug[7]), .DL_Debug(DL_Debug[7]),
    .DL_ADL_73e48c13(DL_ADL_73e48c13), .DL_ADH_067137e0(DL_ADH_067137e0), .DL_DB_4a6f16a8(DL_DB_4a6f16a8),
    .RD(RD), .DBx(in_14), .Dx(in_22), .PHI1(PHI1), .PHI2(PHI2));
endmodule

module ALU (
  input  PHI2,
  input  NDB_ADD_5826378a,
  input  DB_ADD_49072aec,
  input  L_0_ADD_7d0d5e3b,
  input  SB_ADD_21cc08e7,
  input  ADL_ADD_b3e2e6b8,
  input  ADD_SB06_79b3146b,
  input  ADD_SB7_3b72c6f5,
  input  ADD_ADL_d25cdcd8,
  input  ANDS,
  input  EORS,
  input  ORS,
  input  SRS,
  input  SUMS,
  input  SB_AC_692b76aa,
  input  AC_SB_4f3a8e20,
  input  AC_DB_7461a43f,
  input  SB_DB_92ea0e91,
  input  SB_ADH_3fc727a4,
  input  L_ACIN_e8912140,
  input  L_DAA_9902be4a,
  input  L_DSA_8e87f2a8,
  input  in_23,
  input  in_24,
  input  [7:0] ADL_In,
  input  in_26,
  input  DB1,
  input  [7:0] ADH_In,
  input  SB2,
  input  in_30,
  input  SB3,
  input  DB3,
  input  in_33,
  input  in_34,
  input  in_35,
  input  DB5,
  input  in_37,
  input  in_38,
  input  in_39,
  input  in_40,
  output ACR,
  output AVR,
  output [7:0] ADD_Debug,
  output [7:0] AC_Debug,
  output [7:0] AI_Debug,
  output [7:0] BI_Debug,
  output SB0,
  output DB0,
  output ADL0,
  output ADH0,
  output SB1,
  output out_52,
  output ADL1,
  output ADH1,
  output out_55,
  output DB2,
  output ADL2,
  output ADH2,
  output out_59,
  output out_60,
  output ADL3,
  output ADH3,
  output SB4,
  output DB4,
  output ADL4,
  output ADH4,
  output SB5,
  output out_68,
  output ADL5,
  output ADH5,
  output SB6,
  output DB6,
  output ADL6,
  output ADH6,
  output SB7,
  output DB7,
  output ADL7,
  output ADH7
);

  wire ACLatch_q, alu_ops_1_carry4, alu_ops_1_carry6, alu_ops_1_l_carry3_b5e291ef,
       alu_ops_1_l_carry7_555ae96c, and_1_out, bcd_carry_1_dc3, bcd_carry_1_dc7, DCLatch_q, nand_1_out,
       nor_1_out, nor_2_out, not_1_out, not_2_out;
  wire [7:0] alu_add_1_l_addx_38cfd932, alu_bcd_1_out0, alu_ops_1_nand0, alu_ops_1_nor0, alu_ops_1_res0,
       alu_ops_1_xor0;

  ALU_OPS alu_ops_1 (
    .BI_Debug(BI_Debug), .L_carry3_b5e291ef(alu_ops_1_l_carry3_b5e291ef),
    .L_carry7_555ae96c(alu_ops_1_l_carry7_555ae96c), .xor2(alu_ops_1_xor0[2]), .xor3(alu_ops_1_xor0[3]),
    .xor4(alu_ops_1_xor0[4]), .xor5(alu_ops_1_xor0[5]), .xor6(alu_ops_1_xor0[6]), .xor7(alu_ops_1_xor0[7]),
    .res0(alu_ops_1_res0[0]), .res1(alu_ops_1_res0[1]), .res2(alu_ops_1_res0[2]), .res3(alu_ops_1_res0[3]),
    .res4(alu_ops_1_res0[4]), .res5(alu_ops_1_res0[5]), .res6(alu_ops_1_res0[6]), .res7(alu_ops_1_res0[7]),
    .carry4(alu_ops_1_carry4), .nor0(alu_ops_1_nor0[0]), .nor1(alu_ops_1_nor0[1]), .nor2(alu_ops_1_nor0[2]),
    .nor3(alu_ops_1_nor0[3]), .nor4(alu_ops_1_nor0[4]), .nor5(alu_ops_1_nor0[5]), .nor6(alu_ops_1_nor0[6]),
    .nor7(alu_ops_1_nor0[7]), .nand0(alu_ops_1_nand0[0]), .carry6(alu_ops_1_carry6),
    .nand1(alu_ops_1_nand0[1]), .nand2(alu_ops_1_nand0[2]), .nand3(alu_ops_1_nand0[3]),
    .nand4(alu_ops_1_nand0[4]), .nand5(alu_ops_1_nand0[5]), .nand6(alu_ops_1_nand0[6]),
    .nand7(alu_ops_1_nand0[7]), .xor0(alu_ops_1_xor0[0]), .xor1(alu_ops_1_xor0[1]), .AI_Debug(AI_Debug),
    .DB_ADD_49072aec(DB_ADD_49072aec), .DB5(DB5), .DB6(in_38), .DB7(in_40), .ADL0(ADL_In[0]),
    .ADL1(ADL_In[1]), .ADL2(ADL_In[2]), .ADL3(ADL_In[3]), .ADL4(ADL_In[4]), .ADL5(ADL_In[5]),
    .L_0_ADD_7d0d5e3b(L_0_ADD_7d0d5e3b), .ADL6(ADL_In[6]), .ADL7(ADL_In[7]),
    .SB_ADD_21cc08e7(SB_ADD_21cc08e7), .ADL_ADD_b3e2e6b8(ADL_ADD_b3e2e6b8), .ANDS(ANDS), .EORS(EORS),
    .ORS(ORS), .SRS(SRS), .SUMS(SUMS), .L_cin_6a761ec0(L_ACIN_e8912140), .DC3(bcd_carry_1_dc3), .SB0(in_23),
    .SB1(in_26), .SB2(SB2), .SB3(SB3), .NDB_ADD_5826378a(NDB_ADD_5826378a), .SB4(in_33), .SB5(in_35),
    .SB6(in_37), .SB7(in_39), .DB0(in_24), .DB1(DB1), .DB2(in_30), .DB3(DB3), .DB4(in_34));
  BCD_CARRY bcd_carry_1 (
    .DC3(bcd_carry_1_dc3), .DC7(bcd_carry_1_dc7), .L_ACIN_e8912140(L_ACIN_e8912140),
    .carry4(alu_ops_1_carry4), .L_DAA_9902be4a(L_DAA_9902be4a), .\nor (alu_ops_1_nor0),
    .\nand (alu_ops_1_nand0), .\xor (alu_ops_1_xor0));
  nand nand_1 (nand_1_out, alu_ops_1_carry6, alu_ops_1_nor0[7]);
  nor nor_1 (nor_1_out, alu_ops_1_carry6, alu_ops_1_l_carry7_555ae96c);
  not not_1 (not_1_out, nor_1_out);
  ALU_ADD alu_add_1 (
    .L_ADDx_38cfd932(alu_add_1_l_addx_38cfd932), .SB0(SB0), .SB1(SB1), .SB2(out_55), .SB3(out_59), .SB4(SB4),
    .SB5(SB5), .SB6(SB6), .SB7(SB7), .ADL0(ADL0), .ADL1(ADL1), .ADL2(ADL2), .ADL3(ADL3), .ADL4(ADL4),
    .ADL5(ADL5), .ADL6(ADL6), .ADL7(ADL7), .ADD_Debug(ADD_Debug), .ADD_SB06_79b3146b(ADD_SB06_79b3146b),
    .ADD_SB7_3b72c6f5(ADD_SB7_3b72c6f5), .ADD_ADL_d25cdcd8(ADD_ADL_d25cdcd8), .PHI2(PHI2),
    .L_res_63ff9e79(alu_ops_1_res0));
  D_latch_6baf82dd DCLatch (.Q(DCLatch_q), .D(bcd_carry_1_dc7), .EN(PHI2));  // open: NOT_Q
  D_latch_6baf82dd ACLatch (.Q(ACLatch_q), .D(not_2_out), .EN(PHI2));  // open: NOT_Q
  not not_2 (not_2_out, alu_ops_1_l_carry7_555ae96c);
  D_latch_6baf82dd AVRLatch (.NOT_Q(AVR), .D(and_1_out), .EN(PHI2));  // open: Q
  and and_1 (and_1_out, nand_1_out, not_1_out);
  nor nor_2 (nor_2_out, DCLatch_q, ACLatch_q);
  not not_3 (ACR, nor_2_out);
  ALU_BCD alu_bcd_1 (
    .out0(alu_bcd_1_out0[0]), .out1(alu_bcd_1_out0[1]), .out2(alu_bcd_1_out0[2]), .out3(alu_bcd_1_out0[3]),
    .out4(alu_bcd_1_out0[4]), .out5(alu_bcd_1_out0[5]), .out6(alu_bcd_1_out0[6]), .out7(alu_bcd_1_out0[7]),
    .ACR(ACR), .L_DAA_9902be4a(L_DAA_9902be4a), .L_DSA_8e87f2a8(L_DSA_8e87f2a8), .SB0(in_23), .SB1(in_26),
    .SB2(SB2), .SB3(SB3), .PHI2(PHI2), .SB4(in_33), .SB5(in_35), .SB6(in_37), .SB7(in_39),
    .L_carry3_b5e291ef(alu_ops_1_l_carry3_b5e291ef), .L_ADDx_38cfd932(alu_add_1_l_addx_38cfd932));
  ALU_AC alu_ac_1 (
    .AC_Debug(AC_Debug), .SB_Out({SB7, SB6, SB5, SB4, out_59, out_55, SB1, SB0}),
    .DB_Out({DB7, DB6, out_68, DB4, out_60, DB2, out_52, DB0}),
    .ADH_Out({ADH7, ADH6, ADH5, ADH4, ADH3, ADH2, ADH1, ADH0}), .PHI2(PHI2), .SB_AC_692b76aa(SB_AC_692b76aa),
    .AC_SB_4f3a8e20(AC_SB_4f3a8e20), .AC_DB_7461a43f(AC_DB_7461a43f), .SB_DB_92ea0e91(SB_DB_92ea0e91),
    .SB_ADH_3fc727a4(SB_ADH_3fc727a4), .SB_In({in_39, in_37, in_35, in_33, SB3, SB2, in_26, in_23}),
    .DB_In({in_40, in_38, DB5, in_34, DB3, in_30, DB1, in_24}), .ADH_In(ADH_In), .ins(alu_bcd_1_out0));

  // Notes on the sheet:
  //   x8
  //   AVR
  //   ACR
  //   x8
  //   x8
endmodule

module PC (
  input  PHI2,
  input  ADL_PCL_0d330abd,
  input  PCL_PCL_effd7227,
  input  PCL_ADL_75837bef,
  input  PCL_DB_8c5417e4,
  input  ADH_PCH_413c8ef5,
  input  PCH_PCH_e0d1ea0f,
  input  PCH_ADH_329c7fb7,
  input  PCH_DB_4d5eb992,
  input  L_1_PC_f7ea2184,
  input  in_11,
  input  ADL1,
  input  in_13,
  input  in_14,
  input  ADL4,
  input  ADL5,
  input  ADL6,
  input  in_18,
  input  ADH0,
  input  in_20,
  input  ADH2,
  input  ADH3,
  input  in_23,
  input  in_24,
  input  in_25,
  input  in_26,
  output DB0,
  output DB1,
  output DB2,
  output DB3,
  output DB4,
  output DB5,
  output DB6,
  output DB7,
  output ADL0,
  output out_36,
  output ADL2,
  output ADL3,
  output out_39,
  output out_40,
  output out_41,
  output ADL7,
  output out_43,
  output ADH1,
  output out_45,
  output out_46,
  output ADH4,
  output ADH5,
  output ADH6,
  output ADH7,
  output [15:0] PC_Debug,
  output [15:0] PCS_Debug
);

  wire pcl_1_pclc;

  PCL pcl_1 (
    .out_17(ADL0), .ADL1(out_36), .ADL2(ADL2), .out_20(ADL3), .ADL4(out_39), .ADL5(out_40), .out_23(out_41),
    .ADL7(ADL7), .DB0(DB0), .DB1(DB1), .DB2(DB2), .DB3(DB3), .DB4(DB4), .DB5(DB5), .DB6(DB6), .DB7(DB7),
    .PCLS_Debug(PCS_Debug[7:0]), .PCL_Debug(PC_Debug[7:0]), .PCLC(pcl_1_pclc), .cin(L_1_PC_f7ea2184),
    .ADL_PCL_0d330abd(ADL_PCL_0d330abd), .PCL_PCL_effd7227(PCL_PCL_effd7227),
    .PCL_ADL_75837bef(PCL_ADL_75837bef), .PCL_DB_8c5417e4(PCL_DB_8c5417e4), .PHI2(PHI2), .ADL0(in_11),
    .in_8(ADL1), .in_9(in_13), .ADL3(in_14), .in_11(ADL4), .in_12(ADL5), .ADL6(ADL6), .in_14(in_18));
  PCH pch_1 (
    .PCH_Debug(PC_Debug[15:8]), .PCHS_Debug(PCS_Debug[15:8]), .out_15(out_43), .ADH1(ADH1), .out_17(out_45),
    .out_18(out_46), .ADH4(ADH4), .ADH5(ADH5), .out_21(ADH6), .ADH7(ADH7), .DB0(DB0), .DB1(DB1), .DB2(DB2),
    .DB3(DB3), .DB4(DB4), .DB5(DB5), .DB6(DB6), .DB7(DB7), .cin(pcl_1_pclc),
    .ADH_PCH_413c8ef5(ADH_PCH_413c8ef5), .PCH_PCH_e0d1ea0f(PCH_PCH_e0d1ea0f),
    .PCH_ADH_329c7fb7(PCH_ADH_329c7fb7), .PCH_DB_4d5eb992(PCH_DB_4d5eb992), .PHI2(PHI2), .ADH0(ADH0),
    .in_8(in_20), .ADH2(ADH2), .ADH3(ADH3), .in_11(in_23), .in_12(in_24), .ADH6(in_25), .in_14(in_26));
endmodule

module ABL_BIT (
  input  PHI1,
  input  PHI2,
  input  ADL_ABL_ccbf1bfb,
  input  ADLx,
  output Ax
);

  wire and_1_out, not1_out;

  and and_1 (and_1_out, PHI1, ADL_ABL_ccbf1bfb);
  not not1 (not1_out, ADLx);
  D_latch_6baf82dd d_latch_6baf82dd_1 (.NOT_Q(Ax), .D(not1_out), .EN(and_1_out));  // open: Q

  // Notes on the sheet:
  //   not used
endmodule

module ABH_BIT (
  input  PHI1,
  input  PHI2,
  input  ADH_ABH_4fac1902,
  input  ADHx,
  output Ax
);

  wire and_1_out, not1_out;

  and and_1 (and_1_out, PHI1, ADH_ABH_4fac1902);
  not not1 (not1_out, ADHx);
  D_latch_6baf82dd d_latch_6baf82dd_1 (.NOT_Q(Ax), .D(not1_out), .EN(and_1_out));  // open: Q

  // Notes on the sheet:
  //   not used
endmodule

module PCL_EVEN_BIT (
  input  PHI2,
  input  cin,
  input  ADL_PCL_0d330abd,
  input  PCL_PCL_effd7227,
  input  PCL_ADL_75837bef,
  input  PCL_DB_8c5417e4,
  input  ADLx,
  output DBx,
  output out_9,
  output cout,
  output sout,
  output PCL_Debug,
  output PCLS_Debug
);

  wire and_1_out, controlled_buffer_1_out, nand_1_out, not_1_out, PCL_qn;

  nor nor_1 (cout, cin, sout);
  assign controlled_buffer_1_out = PCL_PCL_effd7227 ? PCL_Debug : 1'bz;  // Controlled_Buffer controlled_buffer_1
  assign controlled_buffer_1_out = ADL_PCL_0d330abd ? ADLx : 1'bz;  // Controlled_Buffer controlled_buffer_2
  nand nand_1 (nand_1_out, cin, sout);
  not not_1 (not_1_out, cout);
  D_Flip_Flop #(.trigger("falling")) PCL (.D(and_1_out), .clk(PHI2), .Qn(PCL_qn));  // open: Q, preset, reset
  D_Flip_Flop #(.trigger("high")) PCLS (
    .D(controlled_buffer_1_out), .clk(1'b1), .Q(PCLS_Debug), .Qn(sout));  // open: preset, reset
  and and_1 (and_1_out, nand_1_out, not_1_out);
  not not_2 (PCL_Debug, PCL_qn);
  assign DBx = PCL_DB_8c5417e4 ? PCL_Debug : 1'bz;  // Controlled_Buffer controlled_buffer_3
  assign out_9 = PCL_ADL_75837bef ? PCL_Debug : 1'bz;  // Controlled_Buffer controlled_buffer_4

  // Notes on the sheet:
  //   posedge
endmodule

module PCL_ODD_BIT (
  input  PHI2,
  input  cin,
  input  ADL_PCL_0d330abd,
  input  PCL_PCL_effd7227,
  input  PCL_ADL_75837bef,
  input  PCL_DB_8c5417e4,
  input  ADLx,
  output DBx,
  output out_9,
  output cout,
  output sout,
  output PCL_Debug,
  output PCLS_Debug
);

  wire controlled_buffer_1_out, nor_1_out, not_1_out, not_2_out, not_3_out, or_1_out;

  not not_1 (not_1_out, sout);
  nand nand_1 (cout, cin, not_2_out);
  not not_2 (not_2_out, sout);
  nor nor_1 (nor_1_out, cin, not_1_out);
  not not_3 (not_3_out, cout);
  D_Flip_Flop #(.trigger("falling")) PCL (.D(or_1_out), .clk(PHI2), .Qn(PCL_Debug));  // open: Q, preset, reset
  assign controlled_buffer_1_out = PCL_PCL_effd7227 ? PCL_Debug : 1'bz;  // Controlled_Buffer controlled_buffer_1
  D_Flip_Flop #(.trigger("high")) PCLS (
    .D(controlled_buffer_1_out), .clk(1'b1), .Q(PCLS_Debug), .Qn(sout));  // open: preset, reset
  assign controlled_buffer_1_out = ADL_PCL_0d330abd ? ADLx : 1'bz;  // Controlled_Buffer controlled_buffer_2
  or or_1 (or_1_out, nor_1_out, not_3_out);
  assign DBx = PCL_DB_8c5417e4 ? PCL_Debug : 1'bz;  // Controlled_Buffer controlled_buffer_3
  assign out_9 = PCL_ADL_75837bef ? PCL_Debug : 1'bz;  // Controlled_Buffer controlled_buffer_4

  // Notes on the sheet:
  //   posedge
endmodule

module PCH_EVEN_BIT (
  input  PHI2,
  input  cin,
  input  ADH_PCH_413c8ef5,
  input  PCH_PCH_e0d1ea0f,
  input  PCH_ADH_329c7fb7,
  input  PCH_DB_4d5eb992,
  input  ADHx,
  output DBx,
  output out_9,
  output cout,
  output sout,
  output PCH_Debug,
  output PCHS_Debug
);

  wire controlled_buffer_1_out, nor_1_out, not_1_out, not_2_out, not_3_out, or_1_out;

  not not_1 (not_1_out, sout);
  nand nand_1 (cout, cin, not_2_out);
  not not_2 (not_2_out, sout);
  nor nor_1 (nor_1_out, cin, not_1_out);
  not not_3 (not_3_out, cout);
  D_Flip_Flop #(.trigger("falling")) PCH (.D(or_1_out), .clk(PHI2), .Qn(PCH_Debug));  // open: Q, preset, reset
  assign controlled_buffer_1_out = PCH_PCH_e0d1ea0f ? PCH_Debug : 1'bz;  // Controlled_Buffer controlled_buffer_1
  D_Flip_Flop #(.trigger("high")) PCHS (
    .D(controlled_buffer_1_out), .clk(1'b1), .Q(PCHS_Debug), .Qn(sout));  // open: preset, reset
  assign controlled_buffer_1_out = ADH_PCH_413c8ef5 ? ADHx : 1'bz;  // Controlled_Buffer controlled_buffer_2
  or or_1 (or_1_out, nor_1_out, not_3_out);
  assign DBx = PCH_DB_4d5eb992 ? PCH_Debug : 1'bz;  // Controlled_Buffer controlled_buffer_3
  assign out_9 = PCH_ADH_329c7fb7 ? PCH_Debug : 1'bz;  // Controlled_Buffer controlled_buffer_4

  // Notes on the sheet:
  //   posedge
endmodule

module PCH_ODD_BIT (
  input  PHI2,
  input  cin,
  input  ADH_PCH_413c8ef5,
  input  PCH_PCH_e0d1ea0f,
  input  PCH_ADH_329c7fb7,
  input  PCH_DB_4d5eb992,
  input  ADHx,
  output DBx,
  output out_9,
  output cout,
  output sout,
  output PCH_Debug,
  output PCHS_Debug
);

  wire and_1_out, controlled_buffer_1_out, nand_1_out, not_1_out, PCH_qn;

  nor nor_1 (cout, cin, sout);
  assign controlled_buffer_1_out = PCH_PCH_e0d1ea0f ? PCH_Debug : 1'bz;  // Controlled_Buffer controlled_buffer_1
  assign controlled_buffer_1_out = ADH_PCH_413c8ef5 ? ADHx : 1'bz;  // Controlled_Buffer controlled_buffer_2
  nand nand_1 (nand_1_out, cin, sout);
  not not_1 (not_1_out, cout);
  D_Flip_Flop #(.trigger("falling")) PCH (.D(and_1_out), .clk(PHI2), .Qn(PCH_qn));  // open: Q, preset, reset
  D_Flip_Flop #(.trigger("high")) PCHS (
    .D(controlled_buffer_1_out), .clk(1'b1), .Q(PCHS_Debug), .Qn(sout));  // open: preset, reset
  and and_1 (and_1_out, nand_1_out, not_1_out);
  not not_2 (PCH_Debug, PCH_qn);
  assign DBx = PCH_DB_4d5eb992 ? PCH_Debug : 1'bz;  // Controlled_Buffer controlled_buffer_3
  assign out_9 = PCH_ADH_329c7fb7 ? PCH_Debug : 1'bz;  // Controlled_Buffer controlled_buffer_4

  // Notes on the sheet:
  //   posedge
endmodule

module PCL (
  input  PHI2,
  input  cin,
  input  ADL_PCL_0d330abd,
  input  PCL_PCL_effd7227,
  input  PCL_ADL_75837bef,
  input  PCL_DB_8c5417e4,
  input  ADL0,
  input  in_8,
  input  in_9,
  input  ADL3,
  input  in_11,
  input  in_12,
  input  ADL6,
  input  in_14,
  output [7:0] PCL_Debug,
  output [7:0] PCLS_Debug,
  output out_17,
  output ADL1,
  output ADL2,
  output out_20,
  output ADL4,
  output ADL5,
  output out_23,
  output ADL7,
  output DB0,
  output DB1,
  output DB2,
  output DB3,
  output DB4,
  output DB5,
  output DB6,
  output DB7,
  output PCLC
);

  wire _0_cout, _0_sout, _1_cout, _1_sout, _2_cout, _2_sout, _3_cout, _3_sout, _4_cout, _4_sout, _5_cout,
       _5_sout, _6_cout, _6_sout, _7_sout;

  PCL_EVEN_BIT _0 (
    .DBx(DB0), .out_9(out_17), .cout(_0_cout), .sout(_0_sout), .PCL_Debug(PCL_Debug[0]),
    .PCLS_Debug(PCLS_Debug[0]), .cin(cin), .ADL_PCL_0d330abd(ADL_PCL_0d330abd),
    .PCL_PCL_effd7227(PCL_PCL_effd7227), .PCL_ADL_75837bef(PCL_ADL_75837bef),
    .PCL_DB_8c5417e4(PCL_DB_8c5417e4), .ADLx(ADL0), .PHI2(PHI2));
  PCL_ODD_BIT _1 (
    .out_9(ADL1), .cout(_1_cout), .sout(_1_sout), .PCL_Debug(PCL_Debug[1]), .PCLS_Debug(PCLS_Debug[1]),
    .DBx(DB1), .cin(_0_cout), .ADL_PCL_0d330abd(ADL_PCL_0d330abd), .PCL_PCL_effd7227(PCL_PCL_effd7227),
    .PCL_ADL_75837bef(PCL_ADL_75837bef), .PCL_DB_8c5417e4(PCL_DB_8c5417e4), .ADLx(in_8), .PHI2(PHI2));
  PCL_EVEN_BIT _2 (
    .DBx(DB2), .out_9(ADL2), .cout(_2_cout), .sout(_2_sout), .PCL_Debug(PCL_Debug[2]),
    .PCLS_Debug(PCLS_Debug[2]), .cin(_1_cout), .ADL_PCL_0d330abd(ADL_PCL_0d330abd),
    .PCL_PCL_effd7227(PCL_PCL_effd7227), .PCL_ADL_75837bef(PCL_ADL_75837bef),
    .PCL_DB_8c5417e4(PCL_DB_8c5417e4), .ADLx(in_9), .PHI2(PHI2));
  PCL_ODD_BIT _3 (
    .out_9(out_20), .cout(_3_cout), .sout(_3_sout), .PCL_Debug(PCL_Debug[3]), .PCLS_Debug(PCLS_Debug[3]),
    .DBx(DB3), .cin(_2_cout), .ADL_PCL_0d330abd(ADL_PCL_0d330abd), .PCL_PCL_effd7227(PCL_PCL_effd7227),
    .PCL_ADL_75837bef(PCL_ADL_75837bef), .PCL_DB_8c5417e4(PCL_DB_8c5417e4), .ADLx(ADL3), .PHI2(PHI2));
  PCL_EVEN_BIT _4 (
    .DBx(DB4), .out_9(ADL4), .cout(_4_cout), .sout(_4_sout), .PCL_Debug(PCL_Debug[4]),
    .PCLS_Debug(PCLS_Debug[4]), .cin(_3_cout), .ADL_PCL_0d330abd(ADL_PCL_0d330abd),
    .PCL_PCL_effd7227(PCL_PCL_effd7227), .PCL_ADL_75837bef(PCL_ADL_75837bef),
    .PCL_DB_8c5417e4(PCL_DB_8c5417e4), .ADLx(in_11), .PHI2(PHI2));
  PCL_ODD_BIT _5 (
    .out_9(ADL5), .cout(_5_cout), .sout(_5_sout), .PCL_Debug(PCL_Debug[5]), .PCLS_Debug(PCLS_Debug[5]),
    .DBx(DB5), .cin(_4_cout), .ADL_PCL_0d330abd(ADL_PCL_0d330abd), .PCL_PCL_effd7227(PCL_PCL_effd7227),
    .PCL_ADL_75837bef(PCL_ADL_75837bef), .PCL_DB_8c5417e4(PCL_DB_8c5417e4), .ADLx(in_12), .PHI2(PHI2));
  PCL_EVEN_BIT _6 (
    .DBx(DB6), .out_9(out_23), .cout(_6_cout), .sout(_6_sout), .PCL_Debug(PCL_Debug[6]),
    .PCLS_Debug(PCLS_Debug[6]), .cin(_5_cout), .ADL_PCL_0d330abd(ADL_PCL_0d330abd),
    .PCL_PCL_effd7227(PCL_PCL_effd7227), .PCL_ADL_75837bef(PCL_ADL_75837bef),
    .PCL_DB_8c5417e4(PCL_DB_8c5417e4), .ADLx(ADL6), .PHI2(PHI2));
  PCL_ODD_BIT _7 (
    .out_9(ADL7), .sout(_7_sout), .PCL_Debug(PCL_Debug[7]), .PCLS_Debug(PCLS_Debug[7]), .DBx(DB7),
    .cin(_6_cout), .ADL_PCL_0d330abd(ADL_PCL_0d330abd), .PCL_PCL_effd7227(PCL_PCL_effd7227),
    .PCL_ADL_75837bef(PCL_ADL_75837bef), .PCL_DB_8c5417e4(PCL_DB_8c5417e4), .ADLx(in_14), .PHI2(PHI2));  // open: cout
  nor nor_1 (PCLC, _0_sout, _1_sout, _2_sout, _3_sout, cin, _4_sout, _5_sout, _6_sout, _7_sout);
endmodule

module PCH (
  input  PHI2,
  input  cin,
  input  ADH_PCH_413c8ef5,
  input  PCH_PCH_e0d1ea0f,
  input  PCH_ADH_329c7fb7,
  input  PCH_DB_4d5eb992,
  input  ADH0,
  input  in_8,
  input  ADH2,
  input  ADH3,
  input  in_11,
  input  in_12,
  input  ADH6,
  input  in_14,
  output out_15,
  output ADH1,
  output out_17,
  output out_18,
  output ADH4,
  output ADH5,
  output out_21,
  output ADH7,
  output DB0,
  output DB1,
  output DB2,
  output DB3,
  output DB4,
  output DB5,
  output DB6,
  output DB7,
  output [7:0] PCH_Debug,
  output [7:0] PCHS_Debug
);

  wire _0_cout, _0_sout, _1_cout, _1_sout, _2_cout, _2_sout, _3_sout, _4_cout, _5_cout, _6_cout, nor_1_out,
       not_1_out;

  not not_1 (not_1_out, cin);
  PCH_EVEN_BIT _0 (
    .out_9(out_15), .cout(_0_cout), .sout(_0_sout), .PCH_Debug(PCH_Debug[0]), .PCHS_Debug(PCHS_Debug[0]),
    .DBx(DB0), .cin(cin), .ADH_PCH_413c8ef5(ADH_PCH_413c8ef5), .PCH_PCH_e0d1ea0f(PCH_PCH_e0d1ea0f),
    .PCH_ADH_329c7fb7(PCH_ADH_329c7fb7), .PCH_DB_4d5eb992(PCH_DB_4d5eb992), .ADHx(ADH0), .PHI2(PHI2));
  PCH_ODD_BIT _1 (
    .DBx(DB1), .out_9(ADH1), .cout(_1_cout), .sout(_1_sout), .PCH_Debug(PCH_Debug[1]),
    .PCHS_Debug(PCHS_Debug[1]), .cin(_0_cout), .ADH_PCH_413c8ef5(ADH_PCH_413c8ef5),
    .PCH_PCH_e0d1ea0f(PCH_PCH_e0d1ea0f), .PCH_ADH_329c7fb7(PCH_ADH_329c7fb7),
    .PCH_DB_4d5eb992(PCH_DB_4d5eb992), .ADHx(in_8), .PHI2(PHI2));
  PCH_EVEN_BIT _2 (
    .out_9(out_17), .cout(_2_cout), .sout(_2_sout), .PCH_Debug(PCH_Debug[2]), .PCHS_Debug(PCHS_Debug[2]),
    .DBx(DB2), .cin(_1_cout), .ADH_PCH_413c8ef5(ADH_PCH_413c8ef5), .PCH_PCH_e0d1ea0f(PCH_PCH_e0d1ea0f),
    .PCH_ADH_329c7fb7(PCH_ADH_329c7fb7), .PCH_DB_4d5eb992(PCH_DB_4d5eb992), .ADHx(ADH2), .PHI2(PHI2));
  PCH_ODD_BIT _3 (
    .DBx(DB3), .out_9(out_18), .sout(_3_sout), .PCH_Debug(PCH_Debug[3]), .PCHS_Debug(PCHS_Debug[3]),
    .cin(_2_cout), .ADH_PCH_413c8ef5(ADH_PCH_413c8ef5), .PCH_PCH_e0d1ea0f(PCH_PCH_e0d1ea0f),
    .PCH_ADH_329c7fb7(PCH_ADH_329c7fb7), .PCH_DB_4d5eb992(PCH_DB_4d5eb992), .ADHx(ADH3), .PHI2(PHI2));  // open: cout
  PCH_EVEN_BIT _4 (
    .out_9(ADH4), .cout(_4_cout), .PCH_Debug(PCH_Debug[4]), .PCHS_Debug(PCHS_Debug[4]), .DBx(DB4),
    .cin(nor_1_out), .ADH_PCH_413c8ef5(ADH_PCH_413c8ef5), .PCH_PCH_e0d1ea0f(PCH_PCH_e0d1ea0f),
    .PCH_ADH_329c7fb7(PCH_ADH_329c7fb7), .PCH_DB_4d5eb992(PCH_DB_4d5eb992), .ADHx(in_11), .PHI2(PHI2));  // open: sout
  PCH_ODD_BIT _5 (
    .DBx(DB5), .out_9(ADH5), .cout(_5_cout), .PCH_Debug(PCH_Debug[5]), .PCHS_Debug(PCHS_Debug[5]),
    .cin(_4_cout), .ADH_PCH_413c8ef5(ADH_PCH_413c8ef5), .PCH_PCH_e0d1ea0f(PCH_PCH_e0d1ea0f),
    .PCH_ADH_329c7fb7(PCH_ADH_329c7fb7), .PCH_DB_4d5eb992(PCH_DB_4d5eb992), .ADHx(in_12), .PHI2(PHI2));  // open: sout
  PCH_EVEN_BIT _6 (
    .out_9(out_21), .cout(_6_cout), .PCH_Debug(PCH_Debug[6]), .PCHS_Debug(PCHS_Debug[6]), .DBx(DB6),
    .cin(_5_cout), .ADH_PCH_413c8ef5(ADH_PCH_413c8ef5), .PCH_PCH_e0d1ea0f(PCH_PCH_e0d1ea0f),
    .PCH_ADH_329c7fb7(PCH_ADH_329c7fb7), .PCH_DB_4d5eb992(PCH_DB_4d5eb992), .ADHx(ADH6), .PHI2(PHI2));  // open: sout
  PCH_ODD_BIT _7 (
    .DBx(DB7), .out_9(ADH7), .PCH_Debug(PCH_Debug[7]), .PCHS_Debug(PCHS_Debug[7]), .cin(_6_cout),
    .ADH_PCH_413c8ef5(ADH_PCH_413c8ef5), .PCH_PCH_e0d1ea0f(PCH_PCH_e0d1ea0f),
    .PCH_ADH_329c7fb7(PCH_ADH_329c7fb7), .PCH_DB_4d5eb992(PCH_DB_4d5eb992), .ADHx(in_14), .PHI2(PHI2));  // open: cout, sout
  nor nor_1 (nor_1_out, not_1_out, _3_sout);

  // Notes on the sheet:
  //   PCHC
endmodule

module ALU_OPS (
  input  NDB_ADD_5826378a,
  input  DB_ADD_49072aec,
  input  L_0_ADD_7d0d5e3b,
  input  SB_ADD_21cc08e7,
  input  ADL_ADD_b3e2e6b8,
  input  ANDS,
  input  EORS,
  input  ORS,
  input  SRS,
  input  SUMS,
  input  L_cin_6a761ec0,
  input  DC3,
  input  SB0,
  input  SB1,
  input  SB2,
  input  SB3,
  input  SB4,
  input  SB5,
  input  SB6,
  input  SB7,
  input  DB0,
  input  DB1,
  input  DB2,
  input  DB3,
  input  DB4,
  input  DB5,
  input  DB6,
  input  DB7,
  input  ADL0,
  input  ADL1,
  input  ADL2,
  input  ADL3,
  input  ADL4,
  input  ADL5,
  input  ADL6,
  input  ADL7,
  output L_carry3_b5e291ef,
  output carry4,
  output carry6,
  output L_carry7_555ae96c,
  output res0,
  output res1,
  output res2,
  output res3,
  output res4,
  output res5,
  output res6,
  output res7,
  output nor0,
  output nor1,
  output nor2,
  output nor3,
  output nor4,
  output nor5,
  output nor6,
  output nor7,
  output nand0,
  output nand1,
  output nand2,
  output nand3,
  output nand4,
  output nand5,
  output nand6,
  output nand7,
  output xor0,
  output xor1,
  output xor2,
  output xor3,
  output xor4,
  output xor5,
  output xor6,
  output xor7,
  output [7:0] AI_Debug,
  output [7:0] BI_Debug
);

  wire _0_cout, _1_l_cout_e6352728, _2_cout, _5_l_cout_e6352728, and_1_out, not_1_out;

  ALU_EVEN_BIT _0 (
    .AI_Debug(AI_Debug[0]), .BI_Debug(BI_Debug[0]), .L_res_63ff9e79(res0), .cout(_0_cout), .\nor (nor0),
    .\nand (nand0), .\xor (xor0), .DB_ADD_49072aec(DB_ADD_49072aec), .L_0_ADD_7d0d5e3b(L_0_ADD_7d0d5e3b),
    .SB_ADD_21cc08e7(SB_ADD_21cc08e7), .ADL_ADD_b3e2e6b8(ADL_ADD_b3e2e6b8), .ANDS(ANDS), .EORS(EORS),
    .ORS(ORS), .SRS(SRS), .SUMS(SUMS), .L_cin_6a761ec0(L_cin_6a761ec0), .prev_res(nand1), .SBx(SB0),
    .DBx(DB0), .ADLx(ADL0), .NDB_ADD_5826378a(NDB_ADD_5826378a));
  ALU_ODD_BIT _1 (
    .AI_Debug(AI_Debug[1]), .BI_Debug(BI_Debug[1]), .L_res_63ff9e79(res1),
    .L_cout_e6352728(_1_l_cout_e6352728), .\nor (nor1), .\nand (nand1), .\xor (xor1),
    .L_0_ADD_7d0d5e3b(L_0_ADD_7d0d5e3b), .SB_ADD_21cc08e7(SB_ADD_21cc08e7),
    .ADL_ADD_b3e2e6b8(ADL_ADD_b3e2e6b8), .ANDS(ANDS), .EORS(EORS), .ORS(ORS), .SRS(SRS), .SUMS(SUMS),
    .cin(_0_cout), .prev_res(nand2), .SBx(SB1), .NDB_ADD_5826378a(NDB_ADD_5826378a), .DBx(DB1), .ADLx(ADL1),
    .DB_ADD_49072aec(DB_ADD_49072aec));
  ALU_EVEN_BIT _2 (
    .AI_Debug(AI_Debug[2]), .BI_Debug(BI_Debug[2]), .L_res_63ff9e79(res2), .cout(_2_cout), .\nor (nor2),
    .\nand (nand2), .\xor (xor2), .DB_ADD_49072aec(DB_ADD_49072aec), .L_0_ADD_7d0d5e3b(L_0_ADD_7d0d5e3b),
    .SB_ADD_21cc08e7(SB_ADD_21cc08e7), .ADL_ADD_b3e2e6b8(ADL_ADD_b3e2e6b8), .ANDS(ANDS), .EORS(EORS),
    .ORS(ORS), .SRS(SRS), .SUMS(SUMS), .L_cin_6a761ec0(_1_l_cout_e6352728), .prev_res(nand3), .SBx(SB2),
    .DBx(DB2), .ADLx(ADL2), .NDB_ADD_5826378a(NDB_ADD_5826378a));
  ALU_ODD_BIT _3 (
    .AI_Debug(AI_Debug[3]), .BI_Debug(BI_Debug[3]), .L_res_63ff9e79(res3),
    .L_cout_e6352728(L_carry3_b5e291ef), .\nor (nor3), .\nand (nand3), .\xor (xor3),
    .L_0_ADD_7d0d5e3b(L_0_ADD_7d0d5e3b), .SB_ADD_21cc08e7(SB_ADD_21cc08e7),
    .ADL_ADD_b3e2e6b8(ADL_ADD_b3e2e6b8), .ANDS(ANDS), .EORS(EORS), .ORS(ORS), .SRS(SRS), .SUMS(SUMS),
    .cin(_2_cout), .prev_res(nand4), .SBx(SB3), .NDB_ADD_5826378a(NDB_ADD_5826378a), .DBx(DB3), .ADLx(ADL3),
    .DB_ADD_49072aec(DB_ADD_49072aec));
  not not_1 (not_1_out, DC3);
  and and_1 (and_1_out, L_carry3_b5e291ef, not_1_out);
  ALU_EVEN_BIT _4 (
    .AI_Debug(AI_Debug[4]), .BI_Debug(BI_Debug[4]), .L_res_63ff9e79(res4), .cout(carry4), .\nor (nor4),
    .\nand (nand4), .\xor (xor4), .DB_ADD_49072aec(DB_ADD_49072aec), .L_0_ADD_7d0d5e3b(L_0_ADD_7d0d5e3b),
    .SB_ADD_21cc08e7(SB_ADD_21cc08e7), .ADL_ADD_b3e2e6b8(ADL_ADD_b3e2e6b8), .ANDS(ANDS), .EORS(EORS),
    .ORS(ORS), .SRS(SRS), .SUMS(SUMS), .L_cin_6a761ec0(and_1_out), .prev_res(nand5), .SBx(SB4), .DBx(DB4),
    .ADLx(ADL4), .NDB_ADD_5826378a(NDB_ADD_5826378a));
  ALU_ODD_BIT _5 (
    .AI_Debug(AI_Debug[5]), .BI_Debug(BI_Debug[5]), .L_res_63ff9e79(res5),
    .L_cout_e6352728(_5_l_cout_e6352728), .\nor (nor5), .\nand (nand5), .\xor (xor5),
    .L_0_ADD_7d0d5e3b(L_0_ADD_7d0d5e3b), .SB_ADD_21cc08e7(SB_ADD_21cc08e7),
    .ADL_ADD_b3e2e6b8(ADL_ADD_b3e2e6b8), .ANDS(ANDS), .EORS(EORS), .ORS(ORS), .SRS(SRS), .SUMS(SUMS),
    .cin(carry4), .prev_res(nand6), .SBx(SB5), .NDB_ADD_5826378a(NDB_ADD_5826378a), .DBx(DB5), .ADLx(ADL5),
    .DB_ADD_49072aec(DB_ADD_49072aec));
  ALU_EVEN_BIT _6 (
    .AI_Debug(AI_Debug[6]), .BI_Debug(BI_Debug[6]), .L_res_63ff9e79(res6), .cout(carry6), .\nor (nor6),
    .\nand (nand6), .\xor (xor6), .DB_ADD_49072aec(DB_ADD_49072aec), .L_0_ADD_7d0d5e3b(L_0_ADD_7d0d5e3b),
    .SB_ADD_21cc08e7(SB_ADD_21cc08e7), .ADL_ADD_b3e2e6b8(ADL_ADD_b3e2e6b8), .ANDS(ANDS), .EORS(EORS),
    .ORS(ORS), .SRS(SRS), .SUMS(SUMS), .L_cin_6a761ec0(_5_l_cout_e6352728), .prev_res(nand7), .SBx(SB6),
    .DBx(DB6), .ADLx(ADL6), .NDB_ADD_5826378a(NDB_ADD_5826378a));
  ALU_ODD_BIT _7 (
    .AI_Debug(AI_Debug[7]), .BI_Debug(BI_Debug[7]), .L_res_63ff9e79(res7),
    .L_cout_e6352728(L_carry7_555ae96c), .\nor (nor7), .\nand (nand7), .\xor (xor7),
    .L_0_ADD_7d0d5e3b(L_0_ADD_7d0d5e3b), .SB_ADD_21cc08e7(SB_ADD_21cc08e7),
    .ADL_ADD_b3e2e6b8(ADL_ADD_b3e2e6b8), .ANDS(ANDS), .EORS(EORS), .ORS(ORS), .SRS(SRS), .SUMS(SUMS),
    .cin(carry6), .prev_res(1'b1), .SBx(SB7), .NDB_ADD_5826378a(NDB_ADD_5826378a), .DBx(DB7), .ADLx(ADL7),
    .DB_ADD_49072aec(DB_ADD_49072aec));
endmodule

module ALU_EVEN_BIT (
  input  NDB_ADD_5826378a,
  input  DB_ADD_49072aec,
  input  L_0_ADD_7d0d5e3b,
  input  SB_ADD_21cc08e7,
  input  ADL_ADD_b3e2e6b8,
  input  ANDS,
  input  EORS,
  input  ORS,
  input  SRS,
  input  SUMS,
  input  L_cin_6a761ec0,
  input  prev_res,
  input  SBx,
  input  DBx,
  input  ADLx,
  output L_res_63ff9e79,
  output cout,
  output AI_Debug,
  output \nor ,
  output \nand ,
  output BI_Debug,
  output \xor 
);

  wire and_1_out, controlled_buffer_1_out, controlled_buffer_3_out, nand_2_out, nand_3_out, nand_4_out,
       nor_2_out, not_1_out, not_2_out, not_3_out, not_4_out, not_5_out;

  not not_1 (not_1_out, DBx);
  assign controlled_buffer_1_out = L_0_ADD_7d0d5e3b ? 1'b0 : 1'bz;  // Controlled_Buffer controlled_buffer_1
  assign controlled_buffer_1_out = SB_ADD_21cc08e7 ? SBx : 1'bz;  // Controlled_Buffer controlled_buffer_2
  assign controlled_buffer_3_out = DB_ADD_49072aec ? DBx : 1'bz;  // Controlled_Buffer controlled_buffer_3
  assign controlled_buffer_3_out = NDB_ADD_5826378a ? not_1_out : 1'bz;  // Controlled_Buffer controlled_buffer_4
  assign controlled_buffer_3_out = ADL_ADD_b3e2e6b8 ? ADLx : 1'bz;  // Controlled_Buffer controlled_buffer_5
  D_latch_6baf82dd AI (.Q(AI_Debug), .D(controlled_buffer_1_out), .EN(1'b1));  // open: NOT_Q
  D_latch_6baf82dd BI (.Q(BI_Debug), .D(controlled_buffer_3_out), .EN(1'b1));  // open: NOT_Q
  not not_2 (not_2_out, \nor );
  not not_3 (not_3_out, L_cin_6a761ec0);
  nand nand_1 (\nand , AI_Debug, BI_Debug);
  nor nor_1 (\nor , AI_Debug, BI_Debug);
  nand nand_2 (nand_2_out, not_2_out, \nand );
  nand nand_3 (nand_3_out, not_3_out, nand_2_out);
  not not_4 (not_4_out, nor_2_out);
  nor nor_2 (nor_2_out, not_3_out, nand_2_out);
  nand nand_4 (nand_4_out, L_cin_6a761ec0, \nand );
  not not_5 (not_5_out, \nor );
  and and_1 (and_1_out, nand_3_out, not_4_out);
  and and_2 (cout, nand_4_out, not_5_out);
  assign L_res_63ff9e79 = ANDS ? \nand  : 1'bz;  // Controlled_Buffer controlled_buffer_6
  assign L_res_63ff9e79 = ORS ? \nor  : 1'bz;  // Controlled_Buffer controlled_buffer_7
  assign L_res_63ff9e79 = EORS ? nand_2_out : 1'bz;  // Controlled_Buffer controlled_buffer_8
  assign L_res_63ff9e79 = SRS ? prev_res : 1'bz;  // Controlled_Buffer controlled_buffer_9
  assign L_res_63ff9e79 = SUMS ? and_1_out : 1'bz;  // Controlled_Buffer controlled_buffer_10
  not not_6 (\xor , nand_2_out);

  // Notes on the sheet:
  //   xnor
  //   xor
endmodule

module ALU_ODD_BIT (
  input  NDB_ADD_5826378a,
  input  DB_ADD_49072aec,
  input  L_0_ADD_7d0d5e3b,
  input  SB_ADD_21cc08e7,
  input  ADL_ADD_b3e2e6b8,
  input  ANDS,
  input  EORS,
  input  ORS,
  input  SRS,
  input  SUMS,
  input  cin,
  input  prev_res,
  input  SBx,
  input  DBx,
  input  ADLx,
  output L_res_63ff9e79,
  output L_cout_e6352728,
  output AI_Debug,
  output \nor ,
  output \nand ,
  output BI_Debug,
  output \xor 
);

  wire and_1_out, controlled_buffer_1_out, controlled_buffer_3_out, nand_2_out, nand_3_out, nor_3_out,
       not_1_out, not_2_out, not_3_out, not_4_out, not_5_out, not_6_out;

  not not_1 (not_1_out, DBx);
  assign controlled_buffer_1_out = L_0_ADD_7d0d5e3b ? 1'b0 : 1'bz;  // Controlled_Buffer controlled_buffer_1
  assign controlled_buffer_1_out = SB_ADD_21cc08e7 ? SBx : 1'bz;  // Controlled_Buffer controlled_buffer_2
  assign controlled_buffer_3_out = DB_ADD_49072aec ? DBx : 1'bz;  // Controlled_Buffer controlled_buffer_3
  assign controlled_buffer_3_out = NDB_ADD_5826378a ? not_1_out : 1'bz;  // Controlled_Buffer controlled_buffer_4
  assign controlled_buffer_3_out = ADL_ADD_b3e2e6b8 ? ADLx : 1'bz;  // Controlled_Buffer controlled_buffer_5
  D_latch_6baf82dd AI (.Q(AI_Debug), .D(controlled_buffer_1_out), .EN(1'b1));  // open: NOT_Q
  D_latch_6baf82dd BI (.Q(BI_Debug), .D(controlled_buffer_3_out), .EN(1'b1));  // open: NOT_Q
  not not_2 (not_2_out, \nand );
  not not_3 (not_3_out, cin);
  not not_4 (not_4_out, \nor );
  nand nand_1 (\nand , AI_Debug, BI_Debug);
  nor nor_1 (\nor , AI_Debug, BI_Debug);
  nor nor_2 (\xor , not_2_out, \nor );
  nand nand_2 (nand_2_out, not_3_out, \xor );
  not not_5 (not_5_out, nor_3_out);
  nor nor_3 (nor_3_out, not_3_out, \xor );
  nand nand_3 (nand_3_out, cin, not_4_out);
  not not_6 (not_6_out, not_2_out);
  and and_1 (and_1_out, nand_2_out, not_5_out);
  and and_2 (L_cout_e6352728, nand_3_out, not_6_out);
  assign L_res_63ff9e79 = ANDS ? \nand  : 1'bz;  // Controlled_Buffer controlled_buffer_6
  assign L_res_63ff9e79 = ORS ? \nor  : 1'bz;  // Controlled_Buffer controlled_buffer_7
  assign L_res_63ff9e79 = EORS ? \xor  : 1'bz;  // Controlled_Buffer controlled_buffer_8
  assign L_res_63ff9e79 = SRS ? prev_res : 1'bz;  // Controlled_Buffer controlled_buffer_9
  assign L_res_63ff9e79 = SUMS ? and_1_out : 1'bz;  // Controlled_Buffer controlled_buffer_10

  // Notes on the sheet:
  //   xor
  //   xor
endmodule

module BCD_CARRY (
  input  L_ACIN_e8912140,
  input  carry4,
  input  L_DAA_9902be4a,
  input  [7:0] \nor ,
  input  [7:0] \nand ,
  input  [7:0] \xor ,
  output DC3,
  output DC7
);

  wire and_1_out, L_1_3b22cb4c_out, L_2_4a831fe0_out, L_3_16a57085_out, L_4_1_25b9fc84_out, nand_1_out,
       nand_2_out, nor_1_out, nor_2_out, nor_3_out, nor_4_out, nor_5_out, nor_6_out, not_1_out, not_2_out,
       not_3_out, not_4_out, not_5_out, not_6_out, not_7_out, not_8_out, not_9_out, or_1_out, or_2_out;

  nand nand_1 (nand_1_out, L_ACIN_e8912140, \nand [0]);
  not not_1 (not_1_out, \nor [0]);
  not not_2 (not_2_out, \nand [5]);
  not not_3 (not_3_out, \nand [2]);
  not not_4 (not_4_out, \nand [1]);
  and and_1 (and_1_out, nand_1_out, not_1_out);
  nor nor_1 (nor_1_out, not_3_out, \nor [2]);
  nor nor_2 (nor_2_out, and_1_out, nor_1_out, not_4_out, \xor [1]);
  not not_5 (not_5_out, \nand [1]);
  not not_6 (not_6_out, \nand [6]);
  nor L_4_1_25b9fc84 (L_4_1_25b9fc84_out, carry4, not_2_out, \xor [5], \xor [6]);
  nor L_2_4a831fe0 (L_2_4a831fe0_out, not_3_out, \xor [3]);
  nor nor_3 (nor_3_out, L_2_4a831fe0_out, nor_2_out);
  nor L_3_16a57085 (L_3_16a57085_out, \nor [2], nand_2_out);
  nand nand_2 (nand_2_out, not_5_out, and_1_out);
  nor nor_4 (nor_4_out, \xor [7], not_6_out);
  nor nor_5 (nor_5_out, nor_4_out, L_4_1_25b9fc84_out);
  not not_7 (not_7_out, \xor [6]);
  nor nor_6 (nor_6_out, not_7_out, L_1_3b22cb4c_out);
  nand L_1_3b22cb4c (L_1_3b22cb4c_out, not_2_out, carry4);
  or or_1 (or_1_out, nor_3_out, L_3_16a57085_out);
  or or_2 (or_2_out, nor_5_out, nor_6_out);
  and and_2 (DC3, or_1_out, not_8_out);
  not not_8 (not_8_out, L_DAA_9902be4a);
  and and_3 (DC7, or_2_out, not_9_out);
  not not_9 (not_9_out, L_DAA_9902be4a);

  // Notes on the sheet:
  //   c
  //   b
  //   ~(b | c)
  //   a
endmodule

module ALU_ADD (
  input  PHI2,
  input  ADD_SB06_79b3146b,
  input  ADD_SB7_3b72c6f5,
  input  ADD_ADL_d25cdcd8,
  input  [7:0] L_res_63ff9e79,
  output [7:0] L_ADDx_38cfd932,
  output SB0,
  output SB1,
  output SB2,
  output SB3,
  output SB4,
  output SB5,
  output SB6,
  output SB7,
  output ADL0,
  output ADL1,
  output ADL2,
  output ADL3,
  output ADL4,
  output ADL5,
  output ADL6,
  output ADL7,
  output [7:0] ADD_Debug
);

  D_latch_6baf82dd d_latch_6baf82dd_1 (.Q(L_ADDx_38cfd932[0]), .NOT_Q(ADD_Debug[0]), .D(L_res_63ff9e79[0]), .EN(PHI2));
  D_latch_6baf82dd d_latch_6baf82dd_2 (.Q(L_ADDx_38cfd932[1]), .NOT_Q(ADD_Debug[1]), .D(L_res_63ff9e79[1]), .EN(PHI2));
  D_latch_6baf82dd d_latch_6baf82dd_3 (.Q(L_ADDx_38cfd932[2]), .NOT_Q(ADD_Debug[2]), .D(L_res_63ff9e79[2]), .EN(PHI2));
  D_latch_6baf82dd d_latch_6baf82dd_4 (.Q(L_ADDx_38cfd932[3]), .NOT_Q(ADD_Debug[3]), .D(L_res_63ff9e79[3]), .EN(PHI2));
  D_latch_6baf82dd d_latch_6baf82dd_5 (.Q(L_ADDx_38cfd932[4]), .NOT_Q(ADD_Debug[4]), .D(L_res_63ff9e79[4]), .EN(PHI2));
  D_latch_6baf82dd d_latch_6baf82dd_6 (.Q(L_ADDx_38cfd932[5]), .NOT_Q(ADD_Debug[5]), .D(L_res_63ff9e79[5]), .EN(PHI2));
  D_latch_6baf82dd d_latch_6baf82dd_7 (.Q(L_ADDx_38cfd932[6]), .NOT_Q(ADD_Debug[6]), .D(L_res_63ff9e79[6]), .EN(PHI2));
  D_latch_6baf82dd d_latch_6baf82dd_8 (.Q(L_ADDx_38cfd932[7]), .NOT_Q(ADD_Debug[7]), .D(L_res_63ff9e79[7]), .EN(PHI2));
  assign SB0 = ADD_SB06_79b3146b ? ADD_Debug[0] : 1'bz;  // Controlled_Buffer controlled_buffer_1
  assign SB1 = ADD_SB06_79b3146b ? ADD_Debug[1] : 1'bz;  // Controlled_Buffer controlled_buffer_2
  assign SB2 = ADD_SB06_79b3146b ? ADD_Debug[2] : 1'bz;  // Controlled_Buffer controlled_buffer_3
  assign SB3 = ADD_SB06_79b3146b ? ADD_Debug[3] : 1'bz;  // Controlled_Buffer controlled_buffer_4
  assign SB4 = ADD_SB06_79b3146b ? ADD_Debug[4] : 1'bz;  // Controlled_Buffer controlled_buffer_5
  assign SB5 = ADD_SB06_79b3146b ? ADD_Debug[5] : 1'bz;  // Controlled_Buffer controlled_buffer_6
  assign SB6 = ADD_SB06_79b3146b ? ADD_Debug[6] : 1'bz;  // Controlled_Buffer controlled_buffer_7
  assign SB7 = ADD_SB7_3b72c6f5 ? ADD_Debug[7] : 1'bz;  // Controlled_Buffer controlled_buffer_8
  assign ADL0 = ADD_ADL_d25cdcd8 ? ADD_Debug[0] : 1'bz;  // Controlled_Buffer controlled_buffer_9
  assign ADL1 = ADD_ADL_d25cdcd8 ? ADD_Debug[1] : 1'bz;  // Controlled_Buffer controlled_buffer_10
  assign ADL2 = ADD_ADL_d25cdcd8 ? ADD_Debug[2] : 1'bz;  // Controlled_Buffer controlled_buffer_11
  assign ADL3 = ADD_ADL_d25cdcd8 ? ADD_Debug[3] : 1'bz;  // Controlled_Buffer controlled_buffer_12
  assign ADL4 = ADD_ADL_d25cdcd8 ? ADD_Debug[4] : 1'bz;  // Controlled_Buffer controlled_buffer_13
  assign ADL5 = ADD_ADL_d25cdcd8 ? ADD_Debug[5] : 1'bz;  // Controlled_Buffer controlled_buffer_14
  assign ADL6 = ADD_ADL_d25cdcd8 ? ADD_Debug[6] : 1'bz;  // Controlled_Buffer controlled_buffer_15
  assign ADL7 = ADD_ADL_d25cdcd8 ? ADD_Debug[7] : 1'bz;  // Controlled_Buffer controlled_buffer_16
endmodule
module ALU_BCD (
  input  PHI2,
  input  L_carry3_b5e291ef,
  input  ACR,
  input  L_DAA_9902be4a,
  input  L_DSA_8e87f2a8,
  input  SB0,
  input  SB1,
  input  SB2,
  input  SB3,
  input  SB4,
  input  SB5,
  input  SB6,
  input  SB7,
  input  [7:0] L_ADDx_38cfd932,
  output out0,
  output out1,
  output out2,
  output out3,
  output out4,
  output out5,
  output out6,
  output out7
);

  wire and_1_out, and_2_out, and_3_out, and_4_out, daah_latch_not_q, daal_latch_not_q, dsah_latch_not_q,
       dsal_latch_q, nand_1_out, nand_2_out, nand_3_out, nand_4_out, nand_5_out, nand_6_out, nand_7_out,
       nand_8_out, nand_9_out, nand_10_out, nand_11_out, nor_1_out, nor_2_out, nor_3_out, nor_4_out,
       nor_5_out, nor_6_out, nor_7_out, not_1_out, not_2_out, not_3_out, not_4_out, not_5_out, not_6_out,
       not_7_out, not_8_out, not_9_out, not_10_out, not_11_out, not_12_out;

  not not_1 (not_1_out, L_carry3_b5e291ef);
  not not_2 (not_2_out, L_DAA_9902be4a);
  nand nand_1 (nand_1_out, not_2_out, not_1_out);
  nor nor_1 (nor_1_out, not_1_out, L_DSA_8e87f2a8);
  not not_3 (not_3_out, L_DSA_8e87f2a8);
  nor nor_2 (nor_2_out, L_ADDx_38cfd932[1], L_ADDx_38cfd932[2]);
  not not_4 (not_4_out, nor_2_out);
  nand nand_2 (nand_2_out, L_ADDx_38cfd932[1], L_ADDx_38cfd932[2]);
  nand nand_3 (nand_3_out, L_ADDx_38cfd932[5], L_ADDx_38cfd932[6]);
  nor nor_3 (nor_3_out, L_ADDx_38cfd932[5], L_ADDx_38cfd932[6]);
  not not_5 (not_5_out, nor_3_out);
  D_latch_6baf82dd daal_latch (.NOT_Q(daal_latch_not_q), .D(nand_1_out), .EN(PHI2));  // open: Q
  D_latch_6baf82dd daah_latch (.NOT_Q(daah_latch_not_q), .D(not_2_out), .EN(PHI2));  // open: Q
  D_latch_6baf82dd dsal_latch (.Q(dsal_latch_q), .D(nor_1_out), .EN(PHI2));  // open: NOT_Q
  D_latch_6baf82dd dsah_latch (.NOT_Q(dsah_latch_not_q), .D(not_3_out), .EN(PHI2));  // open: Q
  nand nand_4 (nand_4_out, L_ADDx_38cfd932[1], daal_latch_not_q);
  nand nand_5 (nand_5_out, ~L_ADDx_38cfd932[1], dsal_latch_q);  // NAND_Gate
  nand nand_6 (nand_6_out, not_4_out, dsal_latch_q);
  nand nand_7 (nand_7_out, nand_2_out, daal_latch_not_q);
  nand nand_8 (nand_8_out, L_ADDx_38cfd932[5], nor_4_out);
  nand nand_9 (nand_9_out, ~L_ADDx_38cfd932[5], nor_5_out);  // NAND_Gate
  nand nand_10 (nand_10_out, nand_3_out, nor_4_out);
  nand nand_11 (nand_11_out, not_5_out, nor_5_out);
  not not_6 (not_6_out, ACR);
  and and_1 (and_1_out, nand_4_out, nand_5_out);
  and and_2 (and_2_out, nand_6_out, nand_7_out);
  and and_3 (and_3_out, nand_8_out, nand_9_out);
  and and_4 (and_4_out, nand_10_out, nand_11_out);
  nor nor_4 (nor_4_out, not_6_out, daah_latch_not_q);
  nor nor_5 (nor_5_out, ACR, dsah_latch_not_q);
  nor nor_6 (nor_6_out, dsal_latch_q, daal_latch_not_q);
  not not_7 (not_7_out, SB1);
  not not_8 (not_8_out, SB2);
  not not_9 (not_9_out, SB3);
  nor nor_7 (nor_7_out, nor_4_out, nor_5_out);
  not not_10 (not_10_out, SB5);
  not not_11 (not_11_out, SB6);
  not not_12 (not_12_out, SB7);
  xor xor_1 (out1, nor_6_out, not_7_out);
  xor xor_2 (out2, and_1_out, not_8_out);
  xor xor_3 (out3, and_2_out, not_9_out);
  xor xor_4 (out5, nor_7_out, not_10_out);
  xor xor_5 (out6, and_3_out, not_11_out);
  xor xor_6 (out7, and_4_out, not_12_out);

  assign out0 = SB0;
  assign out4 = SB4;

  // Notes on the sheet:
  //   DAAL
  //   DAAL
  //   DAAH
  //   DSAL
  //   DSAH
  //   DSAL
  //   DAAH
  //   DSAH
endmodule

module ALU_AC (
  input  PHI2,
  input  SB_AC_692b76aa,
  input  AC_SB_4f3a8e20,
  input  AC_DB_7461a43f,
  input  SB_DB_92ea0e91,
  input  SB_ADH_3fc727a4,
  input  [7:0] ins,
  input  [7:0] SB_In,
  input  [7:0] DB_In,
  input  [7:0] ADH_In,
  output [7:0] AC_Debug,
  output [7:0] SB_Out,
  output [7:0] DB_Out,
  output [7:0] ADH_Out
);

  wire controlled_buffer_1_out, controlled_buffer_2_out, controlled_buffer_3_out, controlled_buffer_4_out,
       controlled_buffer_5_out, controlled_buffer_6_out, controlled_buffer_7_out, controlled_buffer_8_out;

  assign controlled_buffer_1_out = SB_AC_692b76aa ? ins[0] : 1'bz;  // Controlled_Buffer controlled_buffer_1
  assign controlled_buffer_2_out = SB_AC_692b76aa ? ins[1] : 1'bz;  // Controlled_Buffer controlled_buffer_2
  assign controlled_buffer_3_out = SB_AC_692b76aa ? ins[2] : 1'bz;  // Controlled_Buffer controlled_buffer_3
  assign controlled_buffer_4_out = SB_AC_692b76aa ? ins[3] : 1'bz;  // Controlled_Buffer controlled_buffer_4
  assign controlled_buffer_5_out = SB_AC_692b76aa ? ins[4] : 1'bz;  // Controlled_Buffer controlled_buffer_5
  assign controlled_buffer_6_out = SB_AC_692b76aa ? ins[5] : 1'bz;  // Controlled_Buffer controlled_buffer_6
  assign controlled_buffer_7_out = SB_AC_692b76aa ? ins[6] : 1'bz;  // Controlled_Buffer controlled_buffer_7
  assign controlled_buffer_8_out = SB_AC_692b76aa ? ins[7] : 1'bz;  // Controlled_Buffer controlled_buffer_8
  D_latch_6baf82dd d_latch_6baf82dd_1 (.Q(AC_Debug[0]), .D(controlled_buffer_1_out), .EN(PHI2));  // open: NOT_Q
  D_latch_6baf82dd d_latch_6baf82dd_2 (.Q(AC_Debug[1]), .D(controlled_buffer_2_out), .EN(PHI2));  // open: NOT_Q
  D_latch_6baf82dd d_latch_6baf82dd_3 (.Q(AC_Debug[2]), .D(controlled_buffer_3_out), .EN(PHI2));  // open: NOT_Q
  D_latch_6baf82dd d_latch_6baf82dd_4 (.Q(AC_Debug[3]), .D(controlled_buffer_4_out), .EN(PHI2));  // open: NOT_Q
  D_latch_6baf82dd d_latch_6baf82dd_5 (.Q(AC_Debug[4]), .D(controlled_buffer_5_out), .EN(PHI2));  // open: NOT_Q
  D_latch_6baf82dd d_latch_6baf82dd_6 (.Q(AC_Debug[5]), .D(controlled_buffer_6_out), .EN(PHI2));  // open: NOT_Q
  D_latch_6baf82dd d_latch_6baf82dd_7 (.Q(AC_Debug[6]), .D(controlled_buffer_7_out), .EN(PHI2));  // open: NOT_Q
  D_latch_6baf82dd d_latch_6baf82dd_8 (.Q(AC_Debug[7]), .D(controlled_buffer_8_out), .EN(PHI2));  // open: NOT_Q
  assign DB_Out = SB_DB_92ea0e91 ? SB_In : 8'bz;  // Controlled_Buffer controlled_buffer_9
  assign SB_Out = AC_SB_4f3a8e20 ? AC_Debug : 8'bz;  // Controlled_Buffer controlled_buffer_10
  assign DB_Out = AC_DB_7461a43f ? AC_Debug : 8'bz;  // Controlled_Buffer controlled_buffer_11
  assign ADH_Out = SB_ADH_3fc727a4 ? SB_In : 8'bz;  // Controlled_Buffer controlled_buffer_12
  assign SB_Out = SB_ADH_3fc727a4 ? ADH_In : 8'bz;  // Controlled_Buffer controlled_buffer_13
  assign SB_Out = SB_DB_92ea0e91 ? DB_In : 8'bz;  // Controlled_Buffer controlled_buffer_14
endmodule

module ADD_SB7 (
  input  PHI1,
  input  PHI2,
  input  L_C_OUT_e01a0d59,
  input  L_ready_2ba3d9e7,
  input  SR,
  input  L_ROR_e72329fe,
  output L_ADD_SB7_42ccbd8d
);

  wire cout_latch_not_q, ff_latch1_not_q, ff_latch2_q, multiplexer_1_out, mux_latch1_q, nor_1_out, not_1_out,
       not_2_out, not_3_out, nready_latch_q, sr_latch1_not_q, sr_latch2_q;

  not not_1 (not_1_out, L_C_OUT_e01a0d59);
  D_latch_6baf82dd cout_latch (.NOT_Q(cout_latch_not_q), .D(not_1_out), .EN(PHI2));  // open: Q
  D_latch_6baf82dd nready_latch (.Q(nready_latch_q), .D(L_ready_2ba3d9e7), .EN(PHI1));  // open: NOT_Q
  not not_2 (not_2_out, SR);
  nor nor_1 (nor_1_out, nready_latch_q, not_2_out);
  D_latch_6baf82dd mux_latch1 (.Q(mux_latch1_q), .D(nor_1_out), .EN(PHI2));  // open: NOT_Q
  D_latch_6baf82dd ff_latch2 (.Q(ff_latch2_q), .D(ff_latch1_not_q), .EN(PHI2));  // open: NOT_Q
  D_latch_6baf82dd sr_latch1 (.NOT_Q(sr_latch1_not_q), .D(SR), .EN(PHI2));  // open: Q
  not not_3 (not_3_out, multiplexer_1_out);
  Multiplexer multiplexer_1 (.in0(ff_latch2_q), .in1(cout_latch_not_q), .out(multiplexer_1_out), .sel(mux_latch1_q));
  D_latch_6baf82dd ff_latch1 (.NOT_Q(ff_latch1_not_q), .D(not_3_out), .EN(PHI1));  // open: Q
  D_latch_6baf82dd sr_latch2 (.Q(sr_latch2_q), .D(sr_latch1_not_q), .EN(PHI1));  // open: NOT_Q
  nor nor_2 (L_ADD_SB7_42ccbd8d, ff_latch1_not_q, sr_latch2_q, L_ROR_e72329fe);

  // Notes on the sheet:
  //   FF
endmodule

module PRECHARGE (
  input  [7:0] SB_In,
  input  [7:0] DB_In,
  input  [7:0] ADL_In,
  input  [7:0] ADH_In,
  output [7:0] SB_Out,
  output [7:0] DB_Out,
  output [7:0] ADL_Out,
  output [7:0] ADH_Out
);


  assign ADH_Out = ADH_In;
  assign ADL_Out = ADL_In;
  assign DB_Out = DB_In;
  assign SB_Out = SB_In;

  // Notes on the sheet:
  //   SB_In: pull=up
  //   DB_In: pull=up
  //   ADL_In: pull=up
  //   ADH_In: pull=up
  //   Take into account that the tristate bus inputs are pulled up to 1, to simulate precharge.
endmodule

module CONST_GEN (
  input  L_0_ADL0_372ea1ce,
  input  L_0_ADL1_1828b789,
  input  L_0_ADL2_a1d2ebaa,
  input  [7:0] ADL_In,
  input  L_0_ADH0_8d3f04fb,
  input  L_0_ADH17_42b6e0bd,
  input  [7:0] ADH_In,
  output [7:0] ADL_Out,
  output [7:0] ADH_Out
);

  and and_1 (ADL_Out[0], ADL_In[0], ~L_0_ADL0_372ea1ce);  // AND_Gate
  and and_2 (ADL_Out[1], ADL_In[1], ~L_0_ADL1_1828b789);  // AND_Gate
  and and_3 (ADL_Out[2], ADL_In[2], ~L_0_ADL2_a1d2ebaa);  // AND_Gate
  and and_4 (ADH_Out[0], ADH_In[0], ~L_0_ADH0_8d3f04fb);  // AND_Gate
  and and_5 (ADH_Out[1], ADH_In[1], ~L_0_ADH17_42b6e0bd);  // AND_Gate
  and and_6 (ADH_Out[2], ADH_In[2], ~L_0_ADH17_42b6e0bd);  // AND_Gate
  and and_7 (ADH_Out[3], ADH_In[3], ~L_0_ADH17_42b6e0bd);  // AND_Gate
  and and_8 (ADH_Out[4], ADH_In[4], ~L_0_ADH17_42b6e0bd);  // AND_Gate
  and and_9 (ADH_Out[5], ADH_In[5], ~L_0_ADH17_42b6e0bd);  // AND_Gate
  and and_10 (ADH_Out[6], ADH_In[6], ~L_0_ADH17_42b6e0bd);  // AND_Gate
  and and_11 (ADH_Out[7], ADH_In[7], ~L_0_ADH17_42b6e0bd);  // AND_Gate

  assign ADL_Out[7:3] = ADL_In[7:3];
endmodule
