// Logisim project 2A03_APU.circ as structural Verilog: 44 circuits, main circuit 2A03_APU
module _2A03_APU (
  input  in_1,
  output out_2,
  output out_3,
  output out_4,
  output out_5,
  output out_6,
  output out_7,
  output out_8,
  output out_9,
  output out_10,
  output out_11,
  output out_12,
  output out_13,
  output out_14,
  output out_15,
  output out_16,
  output out_17,
  output out_18,
  output out_19,
  output out_20,
  output out_21,
  output out_22,
  output out_23,
  output out_24
);

  wire ACLK, clk_divider_1_clk_2, clock_1_out, dpcm_channel_1_dmca0, dpcm_channel_1_dmca1,
       dpcm_channel_1_dmca2, dpcm_channel_1_dmca3, dpcm_channel_1_dmca4, dpcm_channel_1_dmca5,
       dpcm_channel_1_dmca6, dpcm_channel_1_dmca7, dpcm_channel_1_dmca8, dpcm_channel_1_dmca9,
       dpcm_channel_1_dmca10, dpcm_channel_1_dmca11, dpcm_channel_1_dmca12, dpcm_channel_1_dmca13,
       dpcm_channel_1_dmca14, dpcm_channel_1_ndmcint, dpcm_channel_1_out_24, dpcm_channel_1_rundmc,
       dpcm_channel_1_z4, lenght_decoder_1_lc0, lenght_decoder_1_lc1, lenght_decoder_1_lc2,
       lenght_decoder_1_lc3, lenght_decoder_1_lc4, lenght_decoder_1_lc5, lenght_decoder_1_lc6,
       lenght_decoder_1_lc7, lfo_1_d6_state, lfo_1_int, nACLK, nLFO1, nLFO2, PHI1, PHI2, RES,
       sprite_dma_1_cpu_ab, sprite_dma_1_dmc_ab, sprite_dma_1_main_buffer_disable__datapads__disable_1,
       sprite_dma_1_r_w__to_r_w_ic_pin, sprite_dma_1_rd, sprite_dma_1_rdy, sprite_dma_1_wr,
       triangle_channel_1_tri_lc, undriven_2, undriven_3, undriven_4, undriven_5, undriven_6, undriven_8,
       W4000, W4001, W4002, W4003, W4004, W4005, W4006, W4007;
  wire [7:0] undriven;
  wire [15:0] undriven_7;

  SQUARE_CHANNEL_1 square_channel_1_1 (
    .ACLK(ACLK), .nACLK(nACLK), .W4004(W4004), .W4005(W4005), .W4006(W4006), .W4007(W4007), .D0(undriven[0]),
    .D1(undriven[1]), .D2(undriven[2]), .D3(undriven[3]), .D4(undriven[4]), .D5(undriven[5]),
    .D6(undriven[6]), .D7(undriven[7]), .NOSQB(undriven_2), .RES(RES), .nLFO1(undriven_3),
    .nLFO2(undriven_4), .SQA0(out_2), .SQA1(out_4), .SQ2(out_6), .SQA3(out_8));
  TRIANGLE_CHANNEL triangle_channel_1 (
    .PHI1(PHI1), .PHI2(PHI2), .ACLK(ACLK), .nACLK(nACLK), .D0(undriven[0]), .D1(undriven[1]),
    .D2(undriven[2]), .D3(undriven[3]), .D4(undriven[4]), .D5(undriven[5]), .D6(undriven[6]),
    .D7(undriven[7]), .RES(RES), .nLFO1(undriven_3), .NOTRI(undriven_5), .TRI0(out_10), .TRI1(out_11),
    .TRI2(out_12), .TRI3(out_13), .TRI_LC(triangle_channel_1_tri_lc));  // open: W4008, W400A, W400B
  NOISE_CHANNEL noise_channel_1 (
    .ACLK(ACLK), .nACLK(nACLK), .D7(undriven[7]), .D6(undriven[6]), .D5(undriven[5]), .D4(undriven[4]),
    .D3(undriven[3]), .D2(undriven[2]), .D1(undriven[1]), .D0(undriven[0]), .Res(RES), .nLFO1(undriven_3),
    .RND0(out_21), .RND1(out_22), .RND2(out_23), .RND3(out_24));  // open: W400E, W400F, NORND, W400C
  LENGHT_DECODER lenght_decoder_1 (
    .D3(undriven[3]), .D4(undriven[4]), .D5(undriven[5]), .D6(undriven[6]), .D7(undriven[7]),
    .LC7(lenght_decoder_1_lc7), .LC6(lenght_decoder_1_lc6), .LC5(lenght_decoder_1_lc5),
    .LC4(lenght_decoder_1_lc4), .LC3(lenght_decoder_1_lc3), .LC2(lenght_decoder_1_lc2),
    .LC1(lenght_decoder_1_lc1), .LC0(lenght_decoder_1_lc0));
  LENGHT_COUNTER lenght_counter_1 (
    .nACLK(nACLK), .LC7(lenght_decoder_1_lc7), .RES(RES), .LC6(lenght_decoder_1_lc6),
    .LC5(lenght_decoder_1_lc5), .LC4(lenght_decoder_1_lc4), .LC3(lenght_decoder_1_lc3),
    .LC2(lenght_decoder_1_lc2), .LC1(lenght_decoder_1_lc1), .LC0(lenght_decoder_1_lc0));  // open: STEP, W4003, HALT, Carry_Out
  LENGHT_COUNTER lenght_counter_2 (
    .nACLK(nACLK), .LC7(lenght_decoder_1_lc7), .RES(RES), .LC6(lenght_decoder_1_lc6),
    .LC5(lenght_decoder_1_lc5), .LC4(lenght_decoder_1_lc4), .LC3(lenght_decoder_1_lc3),
    .LC2(lenght_decoder_1_lc2), .LC1(lenght_decoder_1_lc1), .LC0(lenght_decoder_1_lc0));  // open: STEP, W4003, HALT, Carry_Out
  LENGHT_COUNTER lenght_counter_3 (
    .nACLK(nACLK), .LC7(lenght_decoder_1_lc7), .RES(RES), .LC6(lenght_decoder_1_lc6),
    .LC5(lenght_decoder_1_lc5), .LC4(lenght_decoder_1_lc4), .LC3(lenght_decoder_1_lc3),
    .LC2(lenght_decoder_1_lc2), .LC1(lenght_decoder_1_lc1), .LC0(lenght_decoder_1_lc0));  // open: STEP, W4003, HALT, Carry_Out
  SQUARE_CHANNEL_0 square_channel_0_1 (
    .ACLK(ACLK), .nACLK(nACLK), .W4000(W4000), .W4001(W4001), .W4002(W4002), .W4003(W4003), .D0(undriven[0]),
    .D1(undriven[1]), .D2(undriven[2]), .D3(undriven[3]), .D4(undriven[4]), .D5(undriven[5]),
    .D6(undriven[6]), .D7(undriven[7]), .NOSQA(undriven_6), .RES(RES), .nLFO1(undriven_3),
    .nLFO2(undriven_4), .SQA0(out_3), .SQA1(out_5), .SQ2(out_7), .SQA3(out_9));
  SPRITE_DMA sprite_dma_1 (
    .PHI1(PHI2), .PHI2(PHI1), .ACLK(ACLK), .nACLK(nACLK), .D0(undriven[0]), .D1(undriven[1]),
    .D2(undriven[2]), .D3(undriven[3]), .D4(undriven[4]), .D5(undriven[5]), .D6(undriven[6]),
    .D7(undriven[7]), .RUNDMC(dpcm_channel_1_rundmc), .in_16(dpcm_channel_1_out_24), .Z4(dpcm_channel_1_z4),
    .R_W(undriven_8), .RES(RES), .CPUA0(undriven_7[0]), .CPUA1(undriven_7[1]), .CPUA2(undriven_7[2]),
    .CPUA3(undriven_7[3]), .CPUA4(undriven_7[4]), .CPUA5(undriven_7[5]), .CPUA6(undriven_7[6]),
    .CPUA7(undriven_7[7]), .CPUA8(undriven_7[8]), .CPUA9(undriven_7[9]), .CPUA10(undriven_7[10]),
    .CPUA11(undriven_7[11]), .CPUA12(undriven_7[12]), .CPUA13(undriven_7[13]), .CPUA14(undriven_7[14]),
    .CPUA15(undriven_7[15]), .DMC0(dpcm_channel_1_dmca0), .DMC1(dpcm_channel_1_dmca1),
    .DMC2(dpcm_channel_1_dmca2), .DMC3(dpcm_channel_1_dmca3), .DMC4(dpcm_channel_1_dmca4),
    .DMC5(dpcm_channel_1_dmca5), .DMC6(dpcm_channel_1_dmca6), .DMC7(dpcm_channel_1_dmca7),
    .DMC8(dpcm_channel_1_dmca8), .DMC9(dpcm_channel_1_dmca9), .DMC10(dpcm_channel_1_dmca10),
    .DMC11(dpcm_channel_1_dmca11), .DMC12(dpcm_channel_1_dmca12), .DMC13(dpcm_channel_1_dmca13),
    .DMC14(dpcm_channel_1_dmca14), .R_W__to_R_W_ic_pin(sprite_dma_1_r_w__to_r_w_ic_pin),
    .RD(sprite_dma_1_rd), .WR(sprite_dma_1_wr),
    .Main_buffer_disable__datapads__disable_1(sprite_dma_1_main_buffer_disable__datapads__disable_1),
    .RDY(sprite_dma_1_rdy), .CPU_AB(sprite_dma_1_cpu_ab), .DMC_AB(sprite_dma_1_dmc_ab));  // open: nR4015, W4014, SPRA0, SPRA1, SPRA2, SPRA3, SPRA4, SPRA5, SPRA6, SPRA7, SPRA8, SPRA9, SPRA10, SPRA11, SPRA12, SPRA13, SPRA14, SPRA15, A0, A1, A2, A3, A4, A5, A6, A7, A8, A9, A10, A11, A12, A13, A14, A15
  LENGHT_COUNTER lenght_counter_4 (
    .nACLK(nACLK), .LC7(lenght_decoder_1_lc7), .RES(RES), .LC6(lenght_decoder_1_lc6),
    .LC5(lenght_decoder_1_lc5), .LC4(lenght_decoder_1_lc4), .LC3(lenght_decoder_1_lc3),
    .LC2(lenght_decoder_1_lc2), .LC1(lenght_decoder_1_lc1), .LC0(lenght_decoder_1_lc0));  // open: STEP, W4003, HALT, Carry_Out
  DPCM_CHANNEL dpcm_channel_1 (
    .PHI1(PHI1), .ACLK(ACLK), .nACLK(nACLK), .D0(undriven[0]), .D1(undriven[1]), .D2(undriven[2]),
    .D3(undriven[3]), .D4(undriven[4]), .D5(undriven[5]), .D6(undriven[6]), .D7(undriven[7]),
    .R_W(undriven_8), .Res(RES), .nDMCINT(dpcm_channel_1_ndmcint), .RUNDMC(dpcm_channel_1_rundmc),
    .out_24(dpcm_channel_1_out_24), .Z4(dpcm_channel_1_z4), .DMC0(out_14), .DMC1(out_15), .DMC2(out_16),
    .DMC3(out_17), .DMC4(out_18), .DMC5(out_19), .DMC6(out_20), .DMCA0(dpcm_channel_1_dmca0),
    .DMCA1(dpcm_channel_1_dmca1), .DMCA2(dpcm_channel_1_dmca2), .DMCA3(dpcm_channel_1_dmca3),
    .DMCA4(dpcm_channel_1_dmca4), .DMCA5(dpcm_channel_1_dmca5), .DMCA6(dpcm_channel_1_dmca6),
    .DMCA7(dpcm_channel_1_dmca7), .DMCA8(dpcm_channel_1_dmca8), .DMCA9(dpcm_channel_1_dmca9),
    .DMCA10(dpcm_channel_1_dmca10), .DMCA11(dpcm_channel_1_dmca11), .DMCA12(dpcm_channel_1_dmca12),
    .DMCA13(dpcm_channel_1_dmca13), .DMCA14(dpcm_channel_1_dmca14));  // open: W4010, W4011, W4012, W4013, W4015, nR4015, D4_2, D7_2
  REGISTER_SELECT register_select_1 (
    .PHI1(PHI1), .R_W(undriven_8));  // open: A15, A14, A13, A12, A11, A10, A9, A8, A7, A6, A5, A4, A3, A2, A1, A0, W4000, W4001, W4002, W4003, W4004, W4005, W4006, W4007, W4008, W400A, W400B, W400C, W400E, W400F, W4010, W4011, W4012, W4013, W4014, W4015, W4016, W4017, nR4015, nR4016, nR4017
  Clock clock_1 (.out(clock_1_out));
  LFO lfo_1 (
    .Res(in_1), .DMCINT(dpcm_channel_1_ndmcint), .nLFO1(nLFO1), .nLFO2(nLFO2), .INT(lfo_1_int),
    .D6_State(lfo_1_d6_state), .PHI1(PHI1), .nACLK(nACLK), .ACLK(ACLK));  // open: W4017, D7, D6, nR4015
  ACLK aclk_1 (.CLK(clk_divider_1_clk_2), .RES(in_1), .PHI1(PHI1), .PHI2(PHI2), .ACLK(ACLK), .nACLK(nACLK));
  CLK_DIVIDER clk_divider_1 (.CLK(clock_1_out), .CLK_2(clk_divider_1_clk_2));  // open: PHI2_CPU, nCLK, PHI0_CPU, M2_PIN
  // NOT_Gate not_1 is placed but not wired

  // Notes on the sheet:
  //   2A03 APU
  //   Main buffer disable (datapads)
endmodule

module D_latch (
  input  EN,
  input  D,
  output Q,
  output NOT_Q
);

  D_Flip_Flop #(.trigger("high")) d_ff_1 (.clk(EN), .D(D), .Q(Q), .Qn(NOT_Q));  // open: preset, en, reset
endmodule

module LFO (
  input  ACLK,
  input  nACLK,
  input  PHI1,
  input  W4017,
  input  D7,
  input  D6,
  input  Res,
  input  nR4015,
  input  DMCINT,
  output nLFO1,
  output nLFO2,
  output D6_State,
  output INT
);

  wire and_1_out, and_2_out, and_3_out, and_4_out, d_ff_1_qn, d_ff_2_q, d_ff_3_qn, d_ff_4_q, d_ff_5_qn,
       d_ff_6_q, d_ff_7_q, d_ff_8_q, d_ff_9_q, d_ff_10_q, d_ff_11_q, d_ff_12_q, d_ff_13_q, d_ff_14_q,
       d_ff_15_q, d_ff_16_q, d_ff_17_q, d_ff_18_q, d_ff_19_q, d_ff_20_q, d_ff_21_q, d_ff_22_q, d_ff_23_q,
       d_ff_23_qn, d_ff_24_q, d_ff_24_qn, d_ff_25_q, d_ff_25_qn, d_ff_26_q, d_ff_26_qn, d_ff_27_q,
       d_ff_27_qn, d_ff_28_q, d_ff_28_qn, d_ff_29_q, d_ff_29_qn, d_ff_30_q, d_ff_30_qn, d_ff_31_q,
       d_ff_31_qn, d_ff_32_q, d_ff_32_qn, d_ff_33_q, d_ff_33_qn, d_ff_34_q, d_ff_34_qn, d_ff_35_q,
       d_ff_35_qn, d_ff_36_q, d_ff_36_qn, d_ff_37_q, d_ff_37_qn, d_ff_38_qn, Nor0_out, Nor1_out, Nor2_out,
       Nor3_out, Nor4_out, Nor5_out, nor_1_out, nor_2_out, nor_3_out, nor_4_out, nor_5_out, nor_6_out,
       nor_7_out, nor_8_out, nor_9_out, nor_10_out, nor_11_out, nor_12_out, nor_13_out, nor_14_out,
       nor_15_out, nor_16_out, nor_17_out, not_1_out, not_2_out;

  and and_1 (and_1_out, ACLK, W4017);
  and and_2 (and_2_out, ACLK, W4017);
  D_Flip_Flop #(.trigger("high")) d_ff_1 (.clk(and_1_out), .D(D7), .Qn(d_ff_1_qn));  // open: Q, preset, en, reset
  D_Flip_Flop #(.trigger("high")) d_ff_2 (.clk(and_2_out), .D(D6), .Q(d_ff_2_q));  // open: Qn, preset, en, reset
  nor nor_1 (nor_1_out, nor_3_out, nor_2_out);
  nor nor_2 (nor_2_out, nor_1_out, W4017, Res);
  D_Flip_Flop d_ff_3 (.clk(nACLK), .D(d_ff_1_qn), .Qn(d_ff_3_qn));  // open: Q, preset, en, reset
  D_Flip_Flop d_ff_4 (.clk(nACLK), .D(nor_2_out), .Q(d_ff_4_q));  // open: Qn, preset, en, reset
  nor nor_3 (nor_3_out, ACLK, d_ff_4_q);
  D_Flip_Flop d_ff_5 (.clk(nACLK), .D(nor_2_out), .Qn(d_ff_5_qn));  // open: Q, preset, en, reset
  nor nor_4 (nor_4_out, d_ff_5_qn, Nor2_out, Nor1_out);
  nor nor_5 (nor_5_out, not_1_out, ACLK);
  not not_1 (not_1_out, nor_4_out);
  D_Flip_Flop d_ff_6 (.clk(nACLK), .D(d_ff_1_qn), .Q(d_ff_6_q));  // open: Qn, preset, en, reset
  D_Flip_Flop d_ff_7 (.clk(nACLK), .D(nor_2_out), .Q(d_ff_7_q));  // open: Qn, preset, en, reset
  D_Flip_Flop d_ff_8 (.clk(nor_5_out), .D(nor_13_out), .Q(d_ff_8_q), .preset(nor_6_out));  // open: Qn, en, reset
  D_Flip_Flop d_ff_9 (.clk(nor_5_out), .D(d_ff_23_q), .Q(d_ff_9_q), .preset(nor_6_out));  // open: Qn, en, reset
  D_Flip_Flop d_ff_10 (.clk(nor_5_out), .D(d_ff_24_q), .Q(d_ff_10_q), .preset(nor_6_out));  // open: Qn, en, reset
  D_Flip_Flop d_ff_11 (.clk(nor_5_out), .D(d_ff_25_q), .Q(d_ff_11_q), .preset(nor_6_out));  // open: Qn, en, reset
  D_Flip_Flop d_ff_12 (.clk(nor_5_out), .D(d_ff_26_q), .Q(d_ff_12_q), .preset(nor_6_out));  // open: Qn, en, reset
  D_Flip_Flop d_ff_13 (.clk(nor_5_out), .D(d_ff_27_q), .Q(d_ff_13_q), .preset(nor_6_out));  // open: Qn, en, reset
  D_Flip_Flop d_ff_14 (.clk(nor_5_out), .D(d_ff_28_q), .Q(d_ff_14_q), .preset(nor_6_out));  // open: Qn, en, reset
  D_Flip_Flop d_ff_15 (.clk(nor_5_out), .D(d_ff_29_q), .Q(d_ff_15_q), .preset(nor_6_out));  // open: Qn, en, reset
  D_Flip_Flop d_ff_16 (.clk(nor_5_out), .D(d_ff_30_q), .Q(d_ff_16_q), .preset(nor_6_out));  // open: Qn, en, reset
  D_Flip_Flop d_ff_17 (.clk(nor_5_out), .D(d_ff_31_q), .Q(d_ff_17_q), .preset(nor_6_out));  // open: Qn, en, reset
  D_Flip_Flop d_ff_18 (.clk(nor_5_out), .D(d_ff_32_q), .Q(d_ff_18_q), .preset(nor_6_out));  // open: Qn, en, reset
  D_Flip_Flop d_ff_19 (.clk(nor_5_out), .D(d_ff_33_q), .Q(d_ff_19_q), .preset(nor_6_out));  // open: Qn, en, reset
  D_Flip_Flop d_ff_20 (.clk(nor_5_out), .D(d_ff_34_q), .Q(d_ff_20_q), .preset(nor_6_out));  // open: Qn, en, reset
  D_Flip_Flop d_ff_21 (.clk(nor_5_out), .D(d_ff_35_q), .Q(d_ff_21_q), .preset(nor_6_out));  // open: Qn, en, reset
  D_Flip_Flop d_ff_22 (.clk(nor_5_out), .D(d_ff_36_q), .Q(d_ff_22_q), .preset(nor_6_out));  // open: Qn, en, reset
  nor nor_6 (nor_6_out, ACLK, nor_4_out);
  nor nor_7 (nor_7_out, d_ff_6_q, d_ff_7_q);
  D_Flip_Flop d_ff_23 (.clk(nACLK), .D(d_ff_8_q), .Q(d_ff_23_q), .Qn(d_ff_23_qn));  // open: preset, en, reset
  D_Flip_Flop d_ff_24 (.clk(nACLK), .D(d_ff_9_q), .Q(d_ff_24_q), .Qn(d_ff_24_qn));  // open: preset, en, reset
  D_Flip_Flop d_ff_25 (.clk(nACLK), .D(d_ff_10_q), .Q(d_ff_25_q), .Qn(d_ff_25_qn));  // open: preset, en, reset
  D_Flip_Flop d_ff_26 (.clk(nACLK), .D(d_ff_11_q), .Q(d_ff_26_q), .Qn(d_ff_26_qn));  // open: preset, en, reset
  D_Flip_Flop d_ff_27 (.clk(nACLK), .D(d_ff_12_q), .Q(d_ff_27_q), .Qn(d_ff_27_qn));  // open: preset, en, reset
  D_Flip_Flop d_ff_28 (.clk(nACLK), .D(d_ff_13_q), .Q(d_ff_28_q), .Qn(d_ff_28_qn));  // open: preset, en, reset
  D_Flip_Flop d_ff_29 (.clk(nACLK), .D(d_ff_14_q), .Q(d_ff_29_q), .Qn(d_ff_29_qn));  // open: preset, en, reset
  D_Flip_Flop d_ff_30 (.clk(nACLK), .D(d_ff_15_q), .Q(d_ff_30_q), .Qn(d_ff_30_qn));  // open: preset, en, reset
  D_Flip_Flop d_ff_31 (.clk(nACLK), .D(d_ff_16_q), .Q(d_ff_31_q), .Qn(d_ff_31_qn));  // open: preset, en, reset
  D_Flip_Flop d_ff_32 (.clk(nACLK), .D(d_ff_17_q), .Q(d_ff_32_q), .Qn(d_ff_32_qn));  // open: preset, en, reset
  D_Flip_Flop d_ff_33 (.clk(nACLK), .D(d_ff_18_q), .Q(d_ff_33_q), .Qn(d_ff_33_qn));  // open: preset, en, reset
  D_Flip_Flop d_ff_34 (.clk(nACLK), .D(d_ff_19_q), .Q(d_ff_34_q), .Qn(d_ff_34_qn));  // open: preset, en, reset
  D_Flip_Flop d_ff_35 (.clk(nACLK), .D(d_ff_20_q), .Q(d_ff_35_q), .Qn(d_ff_35_qn));  // open: preset, en, reset
  D_Flip_Flop d_ff_36 (.clk(nACLK), .D(d_ff_21_q), .Q(d_ff_36_q), .Qn(d_ff_36_qn));  // open: preset, en, reset
  D_Flip_Flop d_ff_37 (.clk(nACLK), .D(d_ff_22_q), .Q(d_ff_37_q), .Qn(d_ff_37_qn));  // open: preset, en, reset
  and and_3 (and_3_out, Nor2_out, d_ff_1_qn);
  nor nor_8 (nor_8_out, PHI1, nR4015);
  nor nor_9 (nor_9_out, and_3_out, nor_10_out);
  nor nor_10 (nor_10_out, nor_9_out, d_ff_2_q, Res, nor_8_out);
  not not_2 (not_2_out, nR4015);
  nor Nor1 (Nor1_out, d_ff_23_qn, d_ff_24_q, d_ff_25_qn, d_ff_26_q, d_ff_27_q, d_ff_28_q, d_ff_29_q, d_ff_30_qn, d_ff_31_qn, d_ff_32_q, d_ff_33_q, d_ff_34_q, d_ff_35_qn, d_ff_36_qn, d_ff_37_qn);
  nor Nor0 (Nor0_out, d_ff_23_q, d_ff_24_q, d_ff_25_q, d_ff_26_q, d_ff_27_q, d_ff_28_q, d_ff_29_q, d_ff_30_q, d_ff_31_q, d_ff_32_q, d_ff_33_q, d_ff_34_q, d_ff_35_q, d_ff_36_q, d_ff_37_q);
  D_Flip_Flop d_ff_38 (.clk(nACLK), .D(nor_9_out), .Qn(d_ff_38_qn));  // open: Q, preset, en, reset
  assign D6_State = not_2_out ? ~d_ff_38_qn : 1'bz;  // Controlled_Inverter controlled_inverter_1
  nor Nor3 (Nor3_out, d_ff_23_qn, d_ff_24_qn, d_ff_25_q, d_ff_26_q, d_ff_27_qn, d_ff_28_q, d_ff_29_qn, d_ff_30_qn, d_ff_31_q, d_ff_32_q, d_ff_33_qn, d_ff_34_qn, d_ff_35_q, d_ff_36_qn, d_ff_37_q);
  nor Nor2 (Nor2_out, d_ff_30_q, d_ff_23_qn, d_ff_24_qn, d_ff_25_qn, d_ff_26_qn, d_ff_27_qn, d_ff_28_q, d_ff_29_q, d_ff_31_q, d_ff_32_qn, d_ff_33_q, d_ff_34_qn, d_ff_35_q, d_ff_36_q, d_ff_37_q, d_ff_3_qn);
  nor Nor5 (Nor5_out, d_ff_23_qn, d_ff_24_q, d_ff_25_q, d_ff_26_q, d_ff_27_q, d_ff_28_qn, d_ff_29_qn, d_ff_30_q, d_ff_31_q, d_ff_32_q, d_ff_33_q, d_ff_34_q, d_ff_35_qn, d_ff_36_q, d_ff_37_q);
  nor Nor4 (Nor4_out, d_ff_23_qn, d_ff_24_qn, d_ff_25_q, d_ff_26_q, d_ff_27_q, d_ff_28_q, d_ff_29_q, d_ff_30_q, d_ff_31_q, d_ff_32_qn, d_ff_33_qn, d_ff_34_q, d_ff_35_qn, d_ff_36_qn, d_ff_37_q);
  nor nor_11 (nor_11_out, Nor0_out, d_ff_37_q, d_ff_36_q);
  and and_4 (and_4_out, d_ff_37_q, d_ff_36_q);
  nor nor_12 (nor_12_out, nor_10_out, DMCINT);
  nor nor_13 (nor_13_out, nor_11_out, and_4_out);
  not not_3 (INT, nor_12_out);
  nor nor_14 (nor_14_out, Nor5_out, Nor4_out, Nor3_out, Nor2_out, Nor1_out, nor_7_out);
  nor nor_15 (nor_15_out, Nor2_out, Nor4_out, Nor1_out, nor_7_out);
  not not_4 (nLFO1, nor_16_out);
  nor nor_16 (nor_16_out, ACLK, nor_14_out);
  nor nor_17 (nor_17_out, ACLK, nor_15_out);
  not not_5 (nLFO2, nor_17_out);

  // Notes on the sheet:
  //   NORFF1
  //   RS2
  //   NORFF2
  //   DL1
  //   DL3
  //   NOR6
  //   DL4
  //   NOR3
  //   INV1
  //   DL6
  //   DL5
  //   NOR1
  //   NOR7
  //   NOR2
  //   0
  //   1
  //   2
  //   3
  //   4
  //   5
  //   6
  //   7
  //   8
  //   9
  //   10
  //   11
  //   12
  //   13
  //   14
  //   NOR4
  //   AND
  //   RS1
  //   NORFF2
  //   NORFF1
  //   DL2
  //   Nor3=11185
  //   Nor2=14914
  //   Nor1=18640
  //   Nor5=3728
  //   Nor4=7456
  //   NOR5
  //   INV2
endmodule

module ACLK (
  input  CLK,
  input  RES,
  output PHI1,
  output PHI2,
  output ACLK,
  output nACLK
);

  wire d_ff_1_qn, d_ff_2_qn, nor_1_out, nor_2_out, not_2_out;

  not not_1 (PHI1, CLK);
  D_Flip_Flop d_ff_1 (.clk(PHI1), .D(nor_1_out), .Qn(d_ff_1_qn));  // open: Q, preset, en, reset
  D_Flip_Flop d_ff_2 (.clk(CLK), .D(d_ff_1_qn), .Qn(d_ff_2_qn));  // open: Q, preset, en, reset
  nor nor_1 (nor_1_out, d_ff_2_qn, RES);
  not not_2 (not_2_out, PHI1);
  nor nor_2 (nor_2_out, nor_1_out, not_2_out);
  nor nor_3 (nACLK, not_2_out, d_ff_2_qn, CLK);
  not not_3 (ACLK, nor_2_out);

  assign PHI2 = CLK;

  // Notes on the sheet:
  //   DL1
  //   DL2
  //   NOR1
  //   INV1
  //   NOR2
  //   NOR3
endmodule

// CLK DIVIDER
module CLK_DIVIDER (
  input  CLK,
  input  PHI2_CPU,
  output CLK_2,
  output nCLK,
  output PHI0_CPU,
  output M2_PIN
);

  wire d_ff_1_qn, d_ff_2_qn, d_ff_3_qn, d_ff_4_qn, d_ff_5_qn, d_ff_6_qn, d_ff_7_qn, d_ff_8_qn, d_ff_9_q,
       d_ff_10_q, d_ff_11_q, d_ff_12_q, nor_3_out, nor_4_out, nor_5_out, nor_6_out, nor_7_out, nor_8_out,
       not_1_out, not_2_out;

  not not_1 (not_1_out, CLK);
  nor nor_1 (CLK_2, not_1_out, nCLK);
  not not_2 (not_2_out, not_1_out);
  D_Flip_Flop d_ff_1 (.clk(nCLK), .D(d_ff_8_qn), .Qn(d_ff_1_qn));  // open: Q, preset, en, reset
  D_Flip_Flop d_ff_2 (.clk(nCLK), .D(nor_3_out), .Qn(d_ff_2_qn));  // open: Q, preset, en, reset
  D_Flip_Flop d_ff_3 (.clk(nCLK), .D(nor_4_out), .Qn(d_ff_3_qn));  // open: Q, preset, en, reset
  D_Flip_Flop d_ff_4 (.clk(nCLK), .D(nor_5_out), .Qn(d_ff_4_qn));  // open: Q, preset, en, reset
  D_Flip_Flop d_ff_5 (.clk(nCLK), .D(nor_6_out), .Qn(d_ff_5_qn));  // open: Q, preset, en, reset
  D_Flip_Flop d_ff_6 (.clk(nCLK), .D(PHI0_CPU), .Qn(d_ff_6_qn));  // open: Q, preset, en, reset
  nor nor_2 (nCLK, CLK_2, not_2_out);
  D_Flip_Flop d_ff_7 (.clk(CLK_2), .D(d_ff_1_qn), .Qn(d_ff_7_qn));  // open: Q, preset, en, reset
  D_Flip_Flop d_ff_8 (.clk(CLK_2), .D(d_ff_2_qn), .Qn(d_ff_8_qn));  // open: Q, preset, en, reset
  D_Flip_Flop d_ff_9 (.clk(CLK_2), .D(d_ff_3_qn), .Q(d_ff_9_q));  // open: Qn, preset, en, reset
  D_Flip_Flop d_ff_10 (.clk(CLK_2), .D(d_ff_4_qn), .Q(d_ff_10_q));  // open: Qn, preset, en, reset
  D_Flip_Flop d_ff_11 (.clk(CLK_2), .D(d_ff_5_qn), .Q(d_ff_11_q));  // open: Qn, preset, en, reset
  D_Flip_Flop d_ff_12 (.clk(CLK_2), .D(d_ff_6_qn), .Q(d_ff_12_q));  // open: Qn, preset, en, reset
  not not_3 (PHI0_CPU, d_ff_7_qn);
  nor nor_3 (nor_3_out, nor_7_out, d_ff_9_q);
  nor nor_4 (nor_4_out, nor_7_out, d_ff_10_q);
  nor nor_5 (nor_5_out, nor_7_out, d_ff_11_q);
  nor nor_6 (nor_6_out, nor_7_out, d_ff_12_q);
  nor nor_7 (nor_7_out, PHI0_CPU, d_ff_8_qn);
  nor nor_8 (nor_8_out, d_ff_2_qn, PHI2_CPU);
  not not_4 (M2_PIN, nor_8_out);

  // Notes on the sheet:
  //   INV1
  //   NOR1
  //   INV2
  //   NOR2
  //   M2 pin is invertor
endmodule

// REGISTER SELECT
module REGISTER_SELECT (
  input  PHI1,
  input  R_W,
  input  A15,
  input  A14,
  input  A13,
  input  A12,
  input  A11,
  input  A10,
  input  A9,
  input  A8,
  input  A7,
  input  A6,
  input  A5,
  input  A4,
  input  A3,
  input  A2,
  input  A1,
  input  A0,
  output W4000,
  output W4001,
  output W4002,
  output W4003,
  output W4004,
  output W4005,
  output W4006,
  output W4007,
  output W4008,
  output W400A,
  output W400B,
  output W400C,
  output W400E,
  output W400F,
  output W4010,
  output W4011,
  output W4012,
  output W4013,
  output W4014,
  output W4015,
  output W4016,
  output W4017,
  output nR4015,
  output nR4016,
  output nR4017
);

  wire nor_1_out, nor_2_out, nor_3_out, nor_4_out, nor_5_out, nor_6_out, nor_7_out, nor_8_out, nor_9_out,
       nor_10_out, nor_11_out, nor_12_out, nor_13_out, nor_14_out, nor_15_out, nor_16_out, nor_17_out,
       nor_18_out, nor_19_out, nor_20_out, nor_21_out, nor_22_out, nor_23_out, nor_24_out, nor_25_out,
       nor_26_out, nor_27_out, not_1_out, not_2_out, not_3_out, not_4_out, not_5_out, not_6_out, not_7_out,
       not_8_out, not_9_out, not_10_out, not_11_out, not_12_out, not_13_out, not_14_out, not_15_out,
       not_16_out, not_17_out, not_18_out, not_19_out, not_20_out, not_21_out, not_22_out, not_23_out,
       not_24_out, not_25_out, not_26_out, not_27_out, not_28_out, not_29_out, not_30_out, not_31_out,
       not_32_out, not_33_out, not_34_out, not_35_out, not_36_out, not_37_out, not_38_out, not_39_out,
       not_40_out, not_41_out, not_42_out, not_43_out, not_44_out, not_45_out, not_46_out, not_47_out,
       not_48_out, not_49_out, not_50_out, not_51_out, not_52_out, not_53_out, not_54_out, not_55_out,
       not_56_out, not_57_out, not_58_out, not_59_out, not_60_out, not_61_out, not_62_out, not_63_out,
       not_64_out, not_65_out, not_66_out, not_67_out, not_68_out, not_69_out, not_70_out, not_71_out,
       not_72_out, not_73_out, not_74_out, not_75_out, not_76_out, not_77_out, not_78_out, not_79_out,
       not_80_out, not_81_out, not_82_out, not_83_out;

  not not_1 (not_1_out, A14);
  not not_2 (not_2_out, R_W);
  nor nor_1 (nor_1_out, A15, not_1_out, A13, A12, A11, A10, A9, A8, A7, A6, A5, R_W);
  nor nor_2 (nor_2_out, A15, not_1_out, A13, A12, A11, A10, A9, A8, A7, A6, A5, not_2_out);
  not not_3 (not_3_out, nor_1_out);
  not not_4 (not_4_out, nor_2_out);
  not not_5 (not_5_out, A0);
  not not_6 (not_6_out, A1);
  not not_7 (not_7_out, A0);
  not not_8 (not_8_out, A1);
  not not_9 (not_9_out, A2);
  not not_10 (not_10_out, A0);
  not not_11 (not_11_out, A2);
  not not_12 (not_12_out, A1);
  not not_13 (not_13_out, A2);
  not not_14 (not_14_out, A0);
  not not_15 (not_15_out, A1);
  not not_16 (not_16_out, A2);
  not not_17 (not_17_out, A3);
  not not_18 (not_18_out, A1);
  not not_19 (not_19_out, A3);
  not not_20 (not_20_out, A0);
  not not_21 (not_21_out, A1);
  not not_22 (not_22_out, A3);
  not not_23 (not_23_out, A2);
  not not_24 (not_24_out, A3);
  not not_25 (not_25_out, A1);
  not not_26 (not_26_out, A2);
  not not_27 (not_27_out, A3);
  not not_28 (not_28_out, A0);
  not not_29 (not_29_out, A1);
  not not_30 (not_30_out, A2);
  not not_31 (not_31_out, A3);
  not not_32 (not_32_out, A4);
  not not_33 (not_33_out, A0);
  not not_34 (not_34_out, A4);
  not not_35 (not_35_out, A1);
  not not_36 (not_36_out, A4);
  not not_37 (not_37_out, A0);
  not not_38 (not_38_out, A1);
  not not_39 (not_39_out, A4);
  not not_40 (not_40_out, A2);
  not not_41 (not_41_out, A4);
  not not_42 (not_42_out, A0);
  not not_43 (not_43_out, A2);
  not not_44 (not_44_out, A4);
  not not_45 (not_45_out, A1);
  not not_46 (not_46_out, A2);
  not not_47 (not_47_out, A4);
  not not_48 (not_48_out, A0);
  not not_49 (not_49_out, A1);
  not not_50 (not_50_out, A2);
  not not_51 (not_51_out, A4);
  not not_52 (not_52_out, A0);
  not not_53 (not_53_out, A2);
  not not_54 (not_54_out, A4);
  not not_55 (not_55_out, A1);
  not not_56 (not_56_out, A2);
  not not_57 (not_57_out, A4);
  not not_58 (not_58_out, A0);
  not not_59 (not_59_out, A1);
  not not_60 (not_60_out, A2);
  not not_61 (not_61_out, A4);
  nor nor_3 (nor_3_out, A0, A1, A2, A3, A4, not_3_out);
  not not_62 (not_62_out, nor_3_out);
  nor nor_4 (nor_4_out, not_5_out, A1, A2, A3, A4, not_3_out);
  not not_63 (not_63_out, nor_4_out);
  not not_64 (not_64_out, nor_5_out);
  nor nor_5 (nor_5_out, A0, not_6_out, A2, A3, A4, not_3_out);
  not not_65 (not_65_out, nor_6_out);
  nor nor_6 (nor_6_out, not_7_out, not_8_out, A2, A3, A4, not_3_out);
  nor nor_7 (nor_7_out, A0, A1, not_9_out, A3, A4, not_3_out);
  not not_66 (not_66_out, nor_7_out);
  nor nor_8 (nor_8_out, not_10_out, A1, not_11_out, A3, A4, not_3_out);
  not not_67 (not_67_out, nor_8_out);
  nor nor_9 (nor_9_out, A0, not_12_out, not_13_out, A3, A4, not_3_out);
  not not_68 (not_68_out, nor_9_out);
  not not_69 (not_69_out, nor_10_out);
  nor nor_10 (nor_10_out, not_14_out, not_15_out, not_16_out, A3, A4, not_3_out);
  not not_70 (not_70_out, nor_11_out);
  nor nor_11 (nor_11_out, A0, A1, A2, not_17_out, A4, not_3_out);
  not not_71 (not_71_out, nor_12_out);
  nor nor_12 (nor_12_out, A0, not_18_out, A2, not_19_out, A4, not_3_out);
  nor nor_13 (nor_13_out, not_20_out, not_21_out, A2, not_22_out, A4, not_3_out);
  not not_72 (not_72_out, nor_13_out);
  nor nor_14 (nor_14_out, A0, A1, not_23_out, not_24_out, A4, not_3_out);
  not not_73 (not_73_out, nor_14_out);
  not not_74 (not_74_out, nor_15_out);
  nor nor_15 (nor_15_out, A0, not_25_out, not_26_out, not_27_out, A4, not_3_out);
  not not_75 (not_75_out, nor_16_out);
  nor nor_16 (nor_16_out, not_28_out, not_29_out, not_30_out, not_31_out, A4, not_3_out);
  nor nor_17 (nor_17_out, A0, A1, A2, A3, not_32_out, not_3_out);
  not not_76 (not_76_out, nor_17_out);
  not not_77 (not_77_out, nor_18_out);
  nor nor_18 (nor_18_out, not_33_out, A1, A2, A3, not_34_out, not_3_out);
  nor nor_19 (nor_19_out, A0, not_35_out, A2, A3, not_36_out, not_3_out);
  not not_78 (not_78_out, nor_19_out);
  nor nor_20 (nor_20_out, not_37_out, not_38_out, A2, A3, not_39_out, not_3_out);
  not not_79 (not_79_out, nor_20_out);
  not not_80 (not_80_out, nor_21_out);
  nor nor_21 (nor_21_out, A0, A1, not_40_out, A3, not_41_out, not_3_out);
  nor nor_22 (nor_22_out, not_42_out, A1, not_43_out, A3, not_44_out, not_3_out);
  not not_81 (not_81_out, nor_22_out);
  not not_82 (not_82_out, nor_23_out);
  nor nor_23 (nor_23_out, A0, not_45_out, not_46_out, A3, not_47_out, not_3_out);
  nor nor_24 (nor_24_out, not_48_out, not_49_out, not_50_out, A3, not_51_out, not_3_out);
  not not_83 (not_83_out, nor_24_out);
  nor nor_25 (nor_25_out, not_52_out, A1, not_53_out, A3, not_54_out, not_4_out);
  not not_84 (nR4015, nor_25_out);
  not not_85 (nR4016, nor_26_out);
  nor nor_26 (nor_26_out, A0, not_55_out, not_56_out, A3, not_57_out, not_4_out);
  nor nor_27 (nor_27_out, not_58_out, not_59_out, not_60_out, A3, not_61_out, not_4_out);
  not not_86 (nR4017, nor_27_out);
  nor nor_28 (W4000, not_62_out, PHI1);
  nor nor_29 (W4001, not_63_out, PHI1);
  nor nor_30 (W4002, not_64_out, PHI1);
  nor nor_31 (W4003, not_65_out, PHI1);
  nor nor_32 (W4004, not_66_out, PHI1);
  nor nor_33 (W4005, not_67_out, PHI1);
  nor nor_34 (W4006, not_68_out, PHI1);
  nor nor_35 (W4007, not_69_out, PHI1);
  nor nor_36 (W4008, not_70_out, PHI1);
  nor nor_37 (W400A, not_71_out, PHI1);
  nor nor_38 (W400B, not_72_out, PHI1);
  nor nor_39 (W400C, not_73_out, PHI1);
  nor nor_40 (W400E, not_74_out, PHI1);
  nor nor_41 (W400F, not_75_out, PHI1);
  nor nor_42 (W4010, not_76_out, PHI1);
  nor nor_43 (W4011, not_77_out, PHI1);
  nor nor_44 (W4012, not_78_out, PHI1);
  nor nor_45 (W4013, not_79_out, PHI1);
  nor nor_46 (W4014, not_80_out, PHI1);
  nor nor_47 (W4015, not_81_out, PHI1);
  nor nor_48 (W4016, not_82_out, PHI1);
  nor nor_49 (W4017, not_83_out, PHI1);

  // Notes on the sheet:
  //   /Enable write ports
endmodule

// SQUARE CHANNEL 1
module SQUARE_CHANNEL_1 (
  input  ACLK,
  input  nACLK,
  input  W4004,
  input  W4005,
  input  W4006,
  input  W4007,
  input  D0,
  input  D1,
  input  D2,
  input  D3,
  input  D4,
  input  D5,
  input  D6,
  input  D7,
  input  NOSQB,
  input  RES,
  input  nLFO1,
  input  nLFO2,
  output SQA0,
  output SQA1,
  output SQ2,
  output SQA3
);

  wire d_ff_1_qn, multiplexer_1_out, multiplexer_2_out, multiplexer_3_out, multiplexer_4_out, nor_1_out,
       not_1_out, not_2_out, not_3_out, not_4_out, not_5_out, square_adder_1_ncout, square_adder_1_pl0,
       square_adder_1_pl1, square_adder_1_pl2, square_adder_1_pl3, square_adder_1_pl4, square_adder_1_pl5,
       square_adder_1_pl6, square_adder_1_pl7, square_adder_1_pl8, square_adder_1_pl9, square_adder_1_pl10,
       square_adder_1_sweep, square_divider_1_fload, square_divider_1_sqout,
       square_envelope_generator_1_env0, square_envelope_generator_1_env1, square_envelope_generator_1_env2,
       square_envelope_generator_1_env3, square_envelope_generator_1_envdis,
       square_envelope_generator_1_vol0, square_envelope_generator_1_vol1, square_envelope_generator_1_vol2,
       square_envelope_generator_1_vol3, square_sweep_control_1_addout, square_sweep_control_1_d_i,
       square_sweep_control_1_sr0, square_sweep_control_1_sr1, square_sweep_control_1_sr2,
       square_sweep_control_1_swctrl, square_sweep_control_1_sweep_2;

  SQUARE_ADDER square_adder_1 (
    .nACLK(nACLK), .ACLK(ACLK), .W4002(W4006), .W4003(W4007), .D0(D0), .D1(D1), .D2(D2), .D3(D3), .D4(D4),
    .D5(D5), .D6(D6), .D7(D7), .Dec_Inc(square_sweep_control_1_d_i), .SR0(square_sweep_control_1_sr0),
    .SR1(square_sweep_control_1_sr1), .SR2(square_sweep_control_1_sr2),
    .Addout(square_sweep_control_1_addout), .PL0(square_adder_1_pl0), .PL1(square_adder_1_pl1),
    .PL2(square_adder_1_pl2), .PL3(square_adder_1_pl3), .PL4(square_adder_1_pl4), .PL5(square_adder_1_pl5),
    .PL6(square_adder_1_pl6), .PL7(square_adder_1_pl7), .PL8(square_adder_1_pl8), .PL9(square_adder_1_pl9),
    .PL10(square_adder_1_pl10), .nCOUT(square_adder_1_ncout), .SWEEP(square_adder_1_sweep));
  SQUARE_SWEEP_CONTROL square_sweep_control_1 (
    .nACLK(nACLK), .ACLK(ACLK), .W4001(W4005), .D0(D0), .D1(D1), .D2(D2), .D3(D3), .D4(D4), .D5(D5), .D6(D6),
    .D7(D7), .nLFO2(nLFO2), .NOSQA(NOSQB), .nCOUT(square_adder_1_ncout), .SWEEP(square_adder_1_sweep),
    .RES(RES), .SR0(square_sweep_control_1_sr0), .SR1(square_sweep_control_1_sr1),
    .SR2(square_sweep_control_1_sr2), .D_I(square_sweep_control_1_d_i),
    .ADDOUT(square_sweep_control_1_addout), .SWEEP_2(square_sweep_control_1_sweep_2),
    .SWCTRL(square_sweep_control_1_swctrl));
  SQUARE_DIVIDER square_divider_1 (
    .nACLK(nACLK), .ACLK(ACLK), .W4000(W4004), .W4003(W4007), .RES(D7), .PL0(square_adder_1_pl0),
    .PL1(square_adder_1_pl1), .PL2(square_adder_1_pl2), .PL3(square_adder_1_pl3), .PL4(square_adder_1_pl4),
    .PL5(square_adder_1_pl5), .PL6(square_adder_1_pl6), .PL7(square_adder_1_pl7), .PL8(square_adder_1_pl8),
    .PL9(square_adder_1_pl9), .PL10(square_adder_1_pl10), .D6(D6), .D7(D7), .FLOAD(square_divider_1_fload),
    .SQOUT(square_divider_1_sqout));
  not not_1 (not_1_out, square_divider_1_sqout);
  nor nor_1 (nor_1_out, not_1_out, NOSQB, square_sweep_control_1_sweep_2, square_sweep_control_1_swctrl);
  D_Flip_Flop d_ff_1 (.clk(nACLK), .D(nor_1_out), .Qn(d_ff_1_qn));  // open: Q, preset, en, reset
  SQUARE_ENVELOPE_GENERATOR square_envelope_generator_1 (
    .nACLK(nACLK), .ACLK(ACLK), .W4000(W4004), .W4003(W4007), .D0(D0), .D1(D1), .D2(D2), .D3(D3), .D4(D4),
    .D5(D5), .nLFO1(nLFO1), .RES(RES), .VOL0(square_envelope_generator_1_vol0),
    .VOL1(square_envelope_generator_1_vol1), .VOL2(square_envelope_generator_1_vol2),
    .VOL3(square_envelope_generator_1_vol3), .ENVDIS(square_envelope_generator_1_envdis),
    .Env0(square_envelope_generator_1_env0), .Env1(square_envelope_generator_1_env1),
    .Env2(square_envelope_generator_1_env2), .Env3(square_envelope_generator_1_env3));
  nor nor_2 (SQA0, not_2_out, d_ff_1_qn);
  nor nor_3 (SQA1, not_3_out, d_ff_1_qn);
  nor nor_4 (SQ2, not_4_out, d_ff_1_qn);
  nor nor_5 (SQA3, not_5_out, d_ff_1_qn);
  not not_2 (not_2_out, multiplexer_1_out);
  Multiplexer #(.enable("false")) multiplexer_1 (
    .in0(square_envelope_generator_1_env0), .in1(square_envelope_generator_1_vol0), .out(multiplexer_1_out),
    .sel(square_envelope_generator_1_envdis));
  not not_3 (not_3_out, multiplexer_2_out);
  Multiplexer #(.enable("false")) multiplexer_2 (
    .in0(square_envelope_generator_1_env1), .in1(square_envelope_generator_1_vol1), .out(multiplexer_2_out),
    .sel(square_envelope_generator_1_envdis));
  Multiplexer #(.enable("false")) multiplexer_3 (
    .in0(square_envelope_generator_1_env2), .in1(square_envelope_generator_1_vol2), .out(multiplexer_3_out),
    .sel(square_envelope_generator_1_envdis));
  not not_4 (not_4_out, multiplexer_3_out);
  Multiplexer #(.enable("false")) multiplexer_4 (
    .in0(square_envelope_generator_1_env3), .in1(square_envelope_generator_1_vol3), .out(multiplexer_4_out),
    .sel(square_envelope_generator_1_envdis));
  not not_5 (not_5_out, multiplexer_4_out);

  // Notes on the sheet:
  //   INV5
  //   DL5
endmodule

// ADDER
module SQUARE_ADDER (
  input  nACLK,
  input  ACLK,
  input  W4002,
  input  W4003,
  input  D0,
  input  D1,
  input  D2,
  input  D3,
  input  D4,
  input  D5,
  input  D6,
  input  D7,
  input  Dec_Inc,
  input  SR0,
  input  SR1,
  input  SR2,
  input  Addout,
  output PL0,
  output PL1,
  output PL2,
  output PL3,
  output PL4,
  output PL5,
  output PL6,
  output PL7,
  output PL8,
  output PL9,
  output PL10,
  output nCOUT,
  output SWEEP
);

  wire not_1_out, square_adder_cell_1_ncarryout, square_adder_cell_1_nsum, square_adder_cell_2_ncarryout,
       square_adder_cell_2_nsum, square_adder_cell_3_ncarryout, square_adder_cell_3_nsum,
       square_adder_cell_4_ncarryout, square_adder_cell_4_nsum, square_adder_cell_5_ncarryout,
       square_adder_cell_5_nsum, square_adder_cell_6_ncarryout, square_adder_cell_6_nsum,
       square_adder_cell_7_ncarryout, square_adder_cell_7_nsum, square_adder_cell_8_ncarryout,
       square_adder_cell_8_nsum, square_adder_cell_9_ncarryout, square_adder_cell_9_nsum,
       square_adder_cell_10_ncarryout, square_adder_cell_10_nsum, square_adder_cell_11_nsum,
       square_barrel_shifter_1_s0, square_barrel_shifter_1_s1, square_barrel_shifter_1_s2,
       square_barrel_shifter_1_s3, square_barrel_shifter_1_s4, square_barrel_shifter_1_s5,
       square_barrel_shifter_1_s6, square_barrel_shifter_1_s7, square_barrel_shifter_1_s8,
       square_barrel_shifter_1_s9, square_barrel_shifter_1_s10, square_register_1_f0, square_register_1_f1,
       square_register_1_f2, square_register_1_f3, square_register_1_f4, square_register_1_f5,
       square_register_1_f6, square_register_1_f7, square_register_1_f8, square_register_1_f9,
       square_register_1_f10, square_register_1_mu0, square_register_1_mu1, square_register_1_mu2,
       square_register_1_mu3, square_register_1_mu4, square_register_1_mu5, square_register_1_mu6,
       square_register_1_mu7, square_register_1_mu8, square_register_1_mu9, square_register_1_mu10,
       square_register_1_nf0, square_register_1_nf1, square_register_1_nf2, square_register_1_nf3,
       square_register_1_nf4, square_register_1_nf5, square_register_1_nf6, square_register_1_nf7,
       square_register_1_nf8, square_register_1_nf9, square_register_1_nf10;

  SQUARE_REGISTER square_register_1 (
    .nACLK(nACLK), .ACLK(ACLK), .W4002(W4002), .W4003(W4003), .D0(D0), .D1(D1), .D2(D2), .D3(D3), .D4(D4),
    .D5(D5), .D6(D6), .D7(D7), .D_I(Dec_Inc), .F0(square_register_1_f0), .nF0(square_register_1_nf0),
    .MU0(square_register_1_mu0), .nSum0(square_adder_cell_1_nsum), .F1(square_register_1_f1),
    .nF1(square_register_1_nf1), .MU1(square_register_1_mu1), .nSum1(square_adder_cell_2_nsum),
    .F2(square_register_1_f2), .nF2(square_register_1_nf2), .MU2(square_register_1_mu2),
    .nSum2(square_adder_cell_3_nsum), .F3(square_register_1_f3), .nF3(square_register_1_nf3),
    .MU3(square_register_1_mu3), .nSum3(square_adder_cell_4_nsum), .F4(square_register_1_f4),
    .nF4(square_register_1_nf4), .MU4(square_register_1_mu4), .nSum4(square_adder_cell_5_nsum),
    .F5(square_register_1_f5), .nF5(square_register_1_nf5), .MU5(square_register_1_mu5),
    .nSum5(square_adder_cell_6_nsum), .F6(square_register_1_f6), .nF6(square_register_1_nf6),
    .MU6(square_register_1_mu6), .nSum6(square_adder_cell_7_nsum), .F7(square_register_1_f7),
    .nF7(square_register_1_nf7), .MU7(square_register_1_mu7), .nSum7(square_adder_cell_8_nsum),
    .F8(square_register_1_f8), .nF8(square_register_1_nf8), .MU8(square_register_1_mu8),
    .nSum8(square_adder_cell_9_nsum), .F9(square_register_1_f9), .nF9(square_register_1_nf9),
    .MU9(square_register_1_mu9), .nSum9(square_adder_cell_10_nsum), .F10(square_register_1_f10),
    .nF10(square_register_1_nf10), .MU10(square_register_1_mu10), .Addout(square_adder_cell_11_nsum),
    .nSum10(Addout));
  SQUARE_BARREL_SHIFTER square_barrel_shifter_1 (
    .MUI0(square_register_1_mu0), .MUI1(square_register_1_mu1), .MUI2(square_register_1_mu2),
    .MUI3(square_register_1_mu3), .MUI4(square_register_1_mu4), .MUI5(square_register_1_mu5),
    .MUI6(square_register_1_mu6), .MUI7(square_register_1_mu7), .MUI8(square_register_1_mu8),
    .MUI9(square_register_1_mu9), .MUI10(square_register_1_mu10), .Dec_Inc(Dec_Inc), .SR0(SR0), .SR1(SR1),
    .SR2(SR2), .S0(square_barrel_shifter_1_s0), .S1(square_barrel_shifter_1_s1),
    .S2(square_barrel_shifter_1_s2), .S3(square_barrel_shifter_1_s3), .S4(square_barrel_shifter_1_s4),
    .S5(square_barrel_shifter_1_s5), .S6(square_barrel_shifter_1_s6), .S7(square_barrel_shifter_1_s7),
    .S8(square_barrel_shifter_1_s8), .S9(square_barrel_shifter_1_s9), .S10(square_barrel_shifter_1_s10));
  not not_1 (not_1_out, Dec_Inc);
  SQUARE_ADDER_CELL square_adder_cell_1 (
    .nCX(1'b1), .FX(square_register_1_f0), .nFX(square_register_1_nf0), .SX(square_barrel_shifter_1_s0),
    .FX_2(PL0), .nSum(square_adder_cell_1_nsum), .nCarryOut(square_adder_cell_1_ncarryout));
  SQUARE_ADDER_CELL square_adder_cell_2 (
    .nCX(square_adder_cell_1_ncarryout), .FX(square_register_1_f1), .nFX(square_register_1_nf1),
    .SX(square_barrel_shifter_1_s1), .FX_2(PL1), .nSum(square_adder_cell_2_nsum),
    .nCarryOut(square_adder_cell_2_ncarryout));
  SQUARE_ADDER_CELL square_adder_cell_3 (
    .nCX(square_adder_cell_2_ncarryout), .FX(square_register_1_f2), .nFX(square_register_1_nf2),
    .SX(square_barrel_shifter_1_s2), .FX_2(PL2), .nSum(square_adder_cell_3_nsum),
    .nCarryOut(square_adder_cell_3_ncarryout));
  SQUARE_ADDER_CELL square_adder_cell_4 (
    .nCX(square_adder_cell_3_ncarryout), .FX(square_register_1_f3), .nFX(square_register_1_nf3),
    .SX(square_barrel_shifter_1_s3), .FX_2(PL3), .nSum(square_adder_cell_4_nsum),
    .nCarryOut(square_adder_cell_4_ncarryout));
  SQUARE_ADDER_CELL square_adder_cell_5 (
    .nCX(square_adder_cell_4_ncarryout), .FX(square_register_1_f4), .nFX(square_register_1_nf4),
    .SX(square_barrel_shifter_1_s4), .FX_2(PL4), .nSum(square_adder_cell_5_nsum),
    .nCarryOut(square_adder_cell_5_ncarryout));
  SQUARE_ADDER_CELL square_adder_cell_6 (
    .nCX(square_adder_cell_5_ncarryout), .FX(square_register_1_f5), .nFX(square_register_1_nf5),
    .SX(square_barrel_shifter_1_s5), .FX_2(PL5), .nSum(square_adder_cell_6_nsum),
    .nCarryOut(square_adder_cell_6_ncarryout));
  SQUARE_ADDER_CELL square_adder_cell_7 (
    .nCX(square_adder_cell_6_ncarryout), .FX(square_register_1_f6), .nFX(square_register_1_nf6),
    .SX(square_barrel_shifter_1_s6), .FX_2(PL6), .nSum(square_adder_cell_7_nsum),
    .nCarryOut(square_adder_cell_7_ncarryout));
  SQUARE_ADDER_CELL square_adder_cell_8 (
    .nCX(square_adder_cell_7_ncarryout), .FX(square_register_1_f7), .nFX(square_register_1_nf7),
    .SX(square_barrel_shifter_1_s7), .FX_2(PL7), .nSum(square_adder_cell_8_nsum),
    .nCarryOut(square_adder_cell_8_ncarryout));
  SQUARE_ADDER_CELL square_adder_cell_9 (
    .nCX(square_adder_cell_8_ncarryout), .FX(square_register_1_f8), .nFX(square_register_1_nf8),
    .SX(square_barrel_shifter_1_s8), .FX_2(PL8), .nSum(square_adder_cell_9_nsum),
    .nCarryOut(square_adder_cell_9_ncarryout));
  SQUARE_ADDER_CELL square_adder_cell_10 (
    .nCX(square_adder_cell_9_ncarryout), .FX(square_register_1_f9), .nFX(square_register_1_nf9),
    .SX(square_barrel_shifter_1_s9), .FX_2(PL9), .nSum(square_adder_cell_10_nsum),
    .nCarryOut(square_adder_cell_10_ncarryout));
  SQUARE_ADDER_CELL square_adder_cell_11 (
    .nCX(square_adder_cell_10_ncarryout), .FX(square_register_1_f10), .nFX(square_register_1_nf10),
    .SX(square_barrel_shifter_1_s10), .FX_2(PL10), .nSum(square_adder_cell_11_nsum), .nCarryOut(nCOUT));
  nor nor_1 (SWEEP, PL2, PL3, PL4, PL5, PL6, PL7, PL8, PL9, PL10);

  // Notes on the sheet:
  //   INC
  //   Connect to VCC for square1, connect to inverter for square2
endmodule

// REGISTER
module SQUARE_REGISTER (
  input  nACLK,
  input  ACLK,
  input  W4002,
  input  W4003,
  input  D0,
  input  nSum0,
  input  D1,
  input  nSum1,
  input  D2,
  input  nSum2,
  input  D3,
  input  nSum3,
  input  D4,
  input  nSum4,
  input  D5,
  input  nSum5,
  input  D6,
  input  nSum6,
  input  D7,
  input  nSum7,
  input  nSum8,
  input  nSum9,
  input  Addout,
  input  nSum10,
  input  D_I,
  output F0,
  output nF0,
  output MU0,
  output F1,
  output nF1,
  output MU1,
  output F2,
  output nF2,
  output MU2,
  output F3,
  output nF3,
  output MU3,
  output F4,
  output nF4,
  output MU4,
  output F5,
  output nF5,
  output MU5,
  output F6,
  output nF6,
  output MU6,
  output F7,
  output nF7,
  output MU7,
  output F8,
  output nF8,
  output MU8,
  output F9,
  output nF9,
  output MU9,
  output F10,
  output nF10,
  output MU10
);

  wire and_1_out, and_2_out, and_3_out, and_4_out, and_5_out, and_6_out, and_7_out, and_8_out, and_9_out,
       and_10_out, and_11_out, and_12_out, and_13_out, and_14_out, and_15_out, and_16_out, and_17_out,
       and_18_out, and_19_out, and_20_out, and_21_out, and_22_out, and_23_out, and_24_out, and_25_out,
       and_26_out, and_27_out, and_28_out, and_29_out, and_30_out, and_31_out, and_32_out, and_33_out,
       d_ff_1_q, d_ff_1_qn, d_ff_2_q, d_ff_2_qn, d_ff_3_q, d_ff_3_qn, d_ff_4_q, d_ff_4_qn, d_ff_5_q,
       d_ff_5_qn, d_ff_6_q, d_ff_6_qn, d_ff_7_q, d_ff_7_qn, d_ff_8_q, d_ff_8_qn, d_ff_9_q, d_ff_9_qn,
       d_ff_10_q, d_ff_10_qn, d_ff_11_q, d_ff_11_qn;

  and and_1 (and_1_out, ACLK, W4002);
  and and_2 (and_2_out, Addout, d_ff_1_q);
  D_Flip_Flop d_ff_1 (.clk(nACLK), .D(nSum0), .Q(d_ff_1_q), .Qn(d_ff_1_qn));  // open: preset, en, reset
  and and_3 (and_3_out, Addout, d_ff_1_qn);
  and and_4 (and_4_out, ACLK, W4002);
  and and_5 (and_5_out, Addout, d_ff_2_q);
  D_Flip_Flop d_ff_2 (.clk(nACLK), .D(nSum1), .Q(d_ff_2_q), .Qn(d_ff_2_qn));  // open: preset, en, reset
  and and_6 (and_6_out, Addout, d_ff_2_qn);
  and and_7 (and_7_out, ACLK, W4002);
  and and_8 (and_8_out, Addout, d_ff_3_q);
  D_Flip_Flop d_ff_3 (.clk(nACLK), .D(nSum2), .Q(d_ff_3_q), .Qn(d_ff_3_qn));  // open: preset, en, reset
  and and_9 (and_9_out, Addout, d_ff_3_qn);
  and and_10 (and_10_out, ACLK, W4002);
  and and_11 (and_11_out, Addout, d_ff_4_q);
  D_Flip_Flop d_ff_4 (.clk(nACLK), .D(nSum3), .Q(d_ff_4_q), .Qn(d_ff_4_qn));  // open: preset, en, reset
  and and_12 (and_12_out, Addout, d_ff_4_qn);
  and and_13 (and_13_out, ACLK, W4002);
  and and_14 (and_14_out, Addout, d_ff_5_q);
  D_Flip_Flop d_ff_5 (.clk(nACLK), .D(nSum4), .Q(d_ff_5_q), .Qn(d_ff_5_qn));  // open: preset, en, reset
  and and_15 (and_15_out, Addout, d_ff_5_qn);
  and and_16 (and_16_out, ACLK, W4002);
  and and_17 (and_17_out, Addout, d_ff_6_q);
  D_Flip_Flop d_ff_6 (.clk(nACLK), .D(nSum5), .Q(d_ff_6_q), .Qn(d_ff_6_qn));  // open: preset, en, reset
  and and_18 (and_18_out, Addout, d_ff_6_qn);
  and and_19 (and_19_out, ACLK, W4002);
  and and_20 (and_20_out, Addout, d_ff_7_q);
  D_Flip_Flop d_ff_7 (.clk(nACLK), .D(nSum6), .Q(d_ff_7_q), .Qn(d_ff_7_qn));  // open: preset, en, reset
  and and_21 (and_21_out, Addout, d_ff_7_qn);
  and and_22 (and_22_out, ACLK, W4002);
  and and_23 (and_23_out, Addout, d_ff_8_q);
  D_Flip_Flop d_ff_8 (.clk(nACLK), .D(nSum7), .Q(d_ff_8_q), .Qn(d_ff_8_qn));  // open: preset, en, reset
  and and_24 (and_24_out, Addout, d_ff_8_qn);
  and and_25 (and_25_out, ACLK, W4003);
  and and_26 (and_26_out, Addout, d_ff_9_q);
  D_Flip_Flop d_ff_9 (.clk(nACLK), .D(nSum8), .Q(d_ff_9_q), .Qn(d_ff_9_qn));  // open: preset, en, reset
  and and_27 (and_27_out, Addout, d_ff_9_qn);
  and and_28 (and_28_out, ACLK, W4003);
  and and_29 (and_29_out, Addout, d_ff_10_q);
  D_Flip_Flop d_ff_10 (.clk(nACLK), .D(nSum9), .Q(d_ff_10_q), .Qn(d_ff_10_qn));  // open: preset, en, reset
  and and_30 (and_30_out, Addout, d_ff_10_qn);
  and and_31 (and_31_out, ACLK, W4003);
  and and_32 (and_32_out, Addout, d_ff_11_q);
  D_Flip_Flop d_ff_11 (.clk(nACLK), .D(nSum10), .Q(d_ff_11_q), .Qn(d_ff_11_qn));  // open: preset, en, reset
  and and_33 (and_33_out, Addout, d_ff_11_qn);
  D_Flip_Flop d_ff_12 (.clk(and_1_out), .D(D0), .Q(F0), .Qn(nF0), .preset(and_3_out), .reset(and_2_out));  // open: en
  D_Flip_Flop d_ff_13 (.clk(and_4_out), .D(D1), .Q(F1), .Qn(nF1), .preset(and_6_out), .reset(and_5_out));  // open: en
  D_Flip_Flop d_ff_14 (.clk(and_7_out), .D(D2), .Q(F2), .Qn(nF2), .preset(and_9_out), .reset(and_8_out));  // open: en
  D_Flip_Flop d_ff_15 (
    .clk(and_10_out), .D(D3), .Q(F3), .Qn(nF3), .preset(and_12_out), .reset(and_11_out));  // open: en
  D_Flip_Flop d_ff_16 (
    .clk(and_13_out), .D(D4), .Q(F4), .Qn(nF4), .preset(and_15_out), .reset(and_14_out));  // open: en
  D_Flip_Flop d_ff_17 (
    .clk(and_16_out), .D(D5), .Q(F5), .Qn(nF5), .preset(and_18_out), .reset(and_17_out));  // open: en
  D_Flip_Flop d_ff_18 (
    .clk(and_19_out), .D(D6), .Q(F6), .Qn(nF6), .preset(and_21_out), .reset(and_20_out));  // open: en
  D_Flip_Flop d_ff_19 (
    .clk(and_22_out), .D(D7), .Q(F7), .Qn(nF7), .preset(and_24_out), .reset(and_23_out));  // open: en
  D_Flip_Flop d_ff_20 (
    .clk(and_25_out), .D(D0), .Q(F8), .Qn(nF8), .preset(and_27_out), .reset(and_26_out));  // open: en
  D_Flip_Flop d_ff_21 (
    .clk(and_28_out), .D(D1), .Q(F9), .Qn(nF9), .preset(and_30_out), .reset(and_29_out));  // open: en
  D_Flip_Flop d_ff_22 (
    .clk(and_31_out), .D(D2), .Q(F10), .Qn(nF10), .preset(and_33_out), .reset(and_32_out));  // open: en
  Multiplexer #(.enable("false")) multiplexer_1 (.in0(F0), .in1(nF0), .out(MU0), .sel(D_I));
  Multiplexer #(.enable("false")) multiplexer_2 (.in0(F1), .in1(nF1), .out(MU1), .sel(D_I));
  Multiplexer #(.enable("false")) multiplexer_3 (.in0(F2), .in1(nF2), .out(MU2), .sel(D_I));
  Multiplexer #(.enable("false")) multiplexer_4 (.in0(F3), .in1(nF3), .out(MU3), .sel(D_I));
  Multiplexer #(.enable("false")) multiplexer_5 (.in0(F4), .in1(nF4), .out(MU4), .sel(D_I));
  Multiplexer #(.enable("false")) multiplexer_6 (.in0(F5), .in1(nF5), .out(MU5), .sel(D_I));
  Multiplexer #(.enable("false")) multiplexer_7 (.in0(F6), .in1(nF6), .out(MU6), .sel(D_I));
  Multiplexer #(.enable("false")) multiplexer_8 (.in0(F7), .in1(nF7), .out(MU7), .sel(D_I));
  Multiplexer #(.enable("false")) multiplexer_9 (.in0(F8), .in1(nF8), .out(MU8), .sel(D_I));
  Multiplexer #(.enable("false")) multiplexer_10 (.in0(F9), .in1(nF9), .out(MU9), .sel(D_I));
  Multiplexer #(.enable("false")) multiplexer_11 (.in0(F10), .in1(nF10), .out(MU10), .sel(D_I));

  // Notes on the sheet:
  //   if /sum 1 reset latch
  //   if /sum 0 preset latch
endmodule

// BARREL SHIFTER
module SQUARE_BARREL_SHIFTER (
  input  MUI0,
  input  MUI1,
  input  MUI2,
  input  MUI3,
  input  MUI4,
  input  MUI5,
  input  MUI6,
  input  MUI7,
  input  MUI8,
  input  MUI9,
  input  MUI10,
  input  Dec_Inc,
  input  SR0,
  input  SR1,
  input  SR2,
  output S0,
  output S1,
  output S2,
  output S3,
  output S4,
  output S5,
  output S6,
  output S7,
  output S8,
  output S9,
  output S10
);

  wire multiplexer_1_out, multiplexer_2_out, multiplexer_3_out, multiplexer_4_out, multiplexer_5_out,
       multiplexer_6_out, multiplexer_7_out, multiplexer_8_out, multiplexer_9_out, multiplexer_10_out,
       multiplexer_11_out, multiplexer_12_out, multiplexer_13_out, multiplexer_14_out, multiplexer_15_out,
       multiplexer_16_out, multiplexer_17_out, multiplexer_18_out, multiplexer_19_out, multiplexer_20_out,
       multiplexer_21_out, multiplexer_22_out;

  Multiplexer #(.enable("false")) multiplexer_1 (.in0(MUI0), .in1(MUI1), .out(multiplexer_1_out), .sel(SR0));
  Multiplexer #(.enable("false")) multiplexer_2 (.in0(MUI1), .in1(MUI2), .out(multiplexer_2_out), .sel(SR0));
  Multiplexer #(.enable("false")) multiplexer_3 (.in0(MUI2), .in1(MUI3), .out(multiplexer_3_out), .sel(SR0));
  Multiplexer #(.enable("false")) multiplexer_4 (.in0(MUI3), .in1(MUI4), .out(multiplexer_4_out), .sel(SR0));
  Multiplexer #(.enable("false")) multiplexer_5 (.in0(MUI4), .in1(MUI5), .out(multiplexer_5_out), .sel(SR0));
  Multiplexer #(.enable("false")) multiplexer_6 (.in0(MUI5), .in1(MUI6), .out(multiplexer_6_out), .sel(SR0));
  Multiplexer #(.enable("false")) multiplexer_7 (.in0(MUI6), .in1(MUI7), .out(multiplexer_7_out), .sel(SR0));
  Multiplexer #(.enable("false")) multiplexer_8 (.in0(MUI7), .in1(MUI8), .out(multiplexer_8_out), .sel(SR0));
  Multiplexer #(.enable("false")) multiplexer_9 (.in0(MUI8), .in1(MUI9), .out(multiplexer_9_out), .sel(SR0));
  Multiplexer #(.enable("false")) multiplexer_10 (.in0(MUI9), .in1(MUI10), .out(multiplexer_10_out), .sel(SR0));
  Multiplexer #(.enable("false")) multiplexer_11 (.in0(MUI10), .in1(Dec_Inc), .out(multiplexer_11_out), .sel(SR0));
  Multiplexer #(.enable("false")) multiplexer_12 (
    .in0(multiplexer_1_out), .in1(multiplexer_3_out), .out(multiplexer_12_out), .sel(SR1));
  Multiplexer #(.enable("false")) multiplexer_13 (
    .in0(multiplexer_2_out), .in1(multiplexer_4_out), .out(multiplexer_13_out), .sel(SR1));
  Multiplexer #(.enable("false")) multiplexer_14 (
    .in0(multiplexer_3_out), .in1(multiplexer_5_out), .out(multiplexer_14_out), .sel(SR1));
  Multiplexer #(.enable("false")) multiplexer_15 (
    .in0(multiplexer_4_out), .in1(multiplexer_6_out), .out(multiplexer_15_out), .sel(SR1));
  Multiplexer #(.enable("false")) multiplexer_16 (
    .in0(multiplexer_5_out), .in1(multiplexer_7_out), .out(multiplexer_16_out), .sel(SR1));
  Multiplexer #(.enable("false")) multiplexer_17 (
    .in0(multiplexer_6_out), .in1(multiplexer_8_out), .out(multiplexer_17_out), .sel(SR1));
  Multiplexer #(.enable("false")) multiplexer_18 (
    .in0(multiplexer_7_out), .in1(multiplexer_9_out), .out(multiplexer_18_out), .sel(SR1));
  Multiplexer #(.enable("false")) multiplexer_19 (
    .in0(multiplexer_8_out), .in1(multiplexer_10_out), .out(multiplexer_19_out), .sel(SR1));
  Multiplexer #(.enable("false")) multiplexer_20 (
    .in0(multiplexer_9_out), .in1(multiplexer_11_out), .out(multiplexer_20_out), .sel(SR1));
  Multiplexer #(.enable("false")) multiplexer_21 (
    .in0(multiplexer_10_out), .in1(Dec_Inc), .out(multiplexer_21_out), .sel(SR1));
  Multiplexer #(.enable("false")) multiplexer_22 (
    .in0(multiplexer_11_out), .in1(Dec_Inc), .out(multiplexer_22_out), .sel(SR1));
  Multiplexer #(.enable("false")) multiplexer_23 (
    .in0(multiplexer_12_out), .in1(multiplexer_16_out), .out(S0), .sel(SR2));
  Multiplexer #(.enable("false")) multiplexer_24 (
    .in0(multiplexer_13_out), .in1(multiplexer_17_out), .out(S1), .sel(SR2));
  Multiplexer #(.enable("false")) multiplexer_25 (
    .in0(multiplexer_14_out), .in1(multiplexer_18_out), .out(S2), .sel(SR2));
  Multiplexer #(.enable("false")) multiplexer_26 (
    .in0(multiplexer_15_out), .in1(multiplexer_19_out), .out(S3), .sel(SR2));
  Multiplexer #(.enable("false")) multiplexer_27 (
    .in0(multiplexer_16_out), .in1(multiplexer_20_out), .out(S4), .sel(SR2));
  Multiplexer #(.enable("false")) multiplexer_28 (
    .in0(multiplexer_17_out), .in1(multiplexer_21_out), .out(S5), .sel(SR2));
  Multiplexer #(.enable("false")) multiplexer_29 (
    .in0(multiplexer_18_out), .in1(multiplexer_22_out), .out(S6), .sel(SR2));
  Multiplexer #(.enable("false")) multiplexer_30 (.in0(multiplexer_19_out), .in1(Dec_Inc), .out(S7), .sel(SR2));
  Multiplexer #(.enable("false")) multiplexer_31 (.in0(multiplexer_20_out), .in1(Dec_Inc), .out(S8), .sel(SR2));
  Multiplexer #(.enable("false")) multiplexer_32 (.in0(multiplexer_21_out), .in1(Dec_Inc), .out(S9), .sel(SR2));
  Multiplexer #(.enable("false")) multiplexer_33 (.in0(multiplexer_22_out), .in1(Dec_Inc), .out(S10), .sel(SR2));

  // Notes on the sheet:
  //   S0
  //   S1
  //   S2
  //   S3
  //   S4
  //   S5
  //   S6
  //   S7
  //   S8
  //   S9
  //   S10
endmodule

module SQUARE_ADDER_CELL (
  input  nCX,
  input  FX,
  input  nFX,
  input  SX,
  output FX_2,
  output nSum,
  output nCarryOut
);

  wire and_1_out, and_2_out, and_3_out, and_4_out, and_5_out, and_6_out, and_7_out, not_1_out, not_2_out;

  not not_1 (not_1_out, nCX);
  not not_2 (not_2_out, SX);
  and and_1 (and_1_out, SX, FX);
  and and_2 (and_2_out, SX, nFX, not_1_out);
  and and_3 (and_3_out, not_2_out, not_1_out, FX);
  nor nor_1 (nCarryOut, and_1_out, and_3_out, and_2_out);
  and and_4 (and_4_out, not_2_out, FX, nCX);
  and and_5 (and_5_out, SX, nFX, nCX);
  and and_6 (and_6_out, not_2_out, nFX, not_1_out);
  nor nor_2 (nSum, and_4_out, and_5_out, and_6_out, and_7_out);
  and and_7 (and_7_out, SX, not_1_out, FX);

  assign FX_2 = FX;

  // Notes on the sheet:
  //   /CX
  //   CX
  //   /FX
  //   /SX
  //   SX
endmodule

// SWEEP CONTROL
module SQUARE_SWEEP_CONTROL (
  input  nACLK,
  input  ACLK,
  input  W4001,
  input  D0,
  input  D1,
  input  D2,
  input  D3,
  input  D4,
  input  D5,
  input  D6,
  input  D7,
  input  nLFO2,
  input  NOSQA,
  input  nCOUT,
  input  SWEEP,
  input  RES,
  output SR0,
  output SR1,
  output SR2,
  output D_I,
  output ADDOUT,
  output SWEEP_2,
  output SWCTRL
);

  wire and_1_out, and_2_out, and_3_out, and_4_out, and_5_out, and_6_out, and_7_out, d_ff_5_q, d_ff_6_q,
       d_ff_7_q, d_ff_8_qn, d_ff_9_q, d_ff_9_qn, d_ff_10_q, d_ff_10_qn, d_ff_11_q, d_ff_11_qn, d_ff_12_qn,
       d_ff_13_q, d_ff_14_qn, d_ff_15_qn, d_ff_16_qn, d_ff_17_qn, d_ff_18_q, multiplexer_1_out,
       multiplexer_2_out, multiplexer_3_out, nor_1_out, nor_2_out, nor_3_out, nor_5_out, nor_6_out,
       nor_7_out, nor_8_out, nor_9_out, nor_10_out, nor_11_out, not_1_out, not_2_out, not_3_out, not_4_out,
       not_5_out, not_6_out, not_7_out, or_1_out, or_2_out, or_3_out;

  and and_1 (and_1_out, ACLK, W4001);
  D_Flip_Flop #(.trigger("high")) d_ff_1 (.clk(and_1_out), .D(D0), .Q(SR0));  // open: Qn, preset, en, reset
  D_Flip_Flop #(.trigger("high")) d_ff_2 (.clk(and_1_out), .D(D1), .Q(SR1));  // open: Qn, preset, en, reset
  D_Flip_Flop #(.trigger("high")) d_ff_3 (.clk(and_1_out), .D(D2), .Q(SR2));  // open: Qn, preset, en, reset
  D_Flip_Flop #(.trigger("high")) d_ff_4 (.clk(and_1_out), .D(D3), .Q(D_I));  // open: Qn, preset, en, reset
  D_Flip_Flop #(.trigger("high")) d_ff_5 (.clk(and_1_out), .D(D4), .Q(d_ff_5_q));  // open: Qn, preset, en, reset
  D_Flip_Flop #(.trigger("high")) d_ff_6 (.clk(and_1_out), .D(D5), .Q(d_ff_6_q));  // open: Qn, preset, en, reset
  D_Flip_Flop #(.trigger("high")) d_ff_7 (.clk(and_1_out), .D(D6), .Q(d_ff_7_q));  // open: Qn, preset, en, reset
  D_Flip_Flop #(.trigger("high")) d_ff_8 (.clk(and_1_out), .D(D7), .Qn(d_ff_8_qn));  // open: Q, preset, en, reset
  nor nor_1 (nor_1_out, nLFO2, d_ff_13_q);
  not not_1 (not_1_out, d_ff_5_q);
  not not_2 (not_2_out, d_ff_6_q);
  not not_3 (not_3_out, d_ff_7_q);
  nor nor_2 (nor_2_out, d_ff_18_q, d_ff_12_qn);
  nor nor_3 (nor_3_out, SR0, SR1, SR2);
  nor nor_4 (SWCTRL, D_I, nCOUT);
  and and_2 (and_2_out, d_ff_5_q, nor_5_out);
  and and_3 (and_3_out, not_1_out, nor_5_out);
  and and_4 (and_4_out, d_ff_6_q, nor_5_out);
  and and_5 (and_5_out, not_2_out, nor_5_out);
  and and_6 (and_6_out, d_ff_7_q, nor_5_out);
  and and_7 (and_7_out, not_3_out, nor_5_out);
  nor nor_5 (nor_5_out, nor_2_out, nLFO2);
  not not_4 (not_4_out, nor_2_out);
  nor nor_6 (nor_6_out, nor_1_out, nor_7_out);
  nor nor_7 (nor_7_out, nor_6_out, W4001);
  D_Flip_Flop d_ff_9 (
    .clk(nor_8_out), .D(d_ff_14_qn), .Q(d_ff_9_q), .Qn(d_ff_9_qn), .preset(and_2_out), .reset(or_1_out));  // open: en
  or or_1 (or_1_out, and_3_out, RES);
  D_Flip_Flop d_ff_10 (
    .clk(nor_8_out), .D(d_ff_15_qn), .Q(d_ff_10_q), .Qn(d_ff_10_qn), .preset(and_4_out), .reset(or_2_out));  // open: en
  or or_2 (or_2_out, and_5_out, RES);
  D_Flip_Flop d_ff_11 (
    .clk(nor_8_out), .D(d_ff_16_qn), .Q(d_ff_11_q), .Qn(d_ff_11_qn), .preset(and_6_out), .reset(or_3_out));  // open: en
  or or_3 (or_3_out, and_7_out, RES);
  nor nor_8 (nor_8_out, not_4_out, nLFO2);
  D_Flip_Flop d_ff_12 (.clk(nACLK), .D(nor_7_out), .Qn(d_ff_12_qn));  // open: Q, preset, en, reset
  D_Flip_Flop d_ff_13 (.clk(nACLK), .Q(d_ff_13_q));  // open: D, Qn, preset, en, reset
  Multiplexer multiplexer_1 (.in0(d_ff_9_qn), .in1(d_ff_9_q), .out(multiplexer_1_out), .sel(1'b1));  // open: en
  not not_5 (not_5_out, 1'b1);
  Multiplexer multiplexer_2 (.in0(d_ff_10_qn), .in1(d_ff_10_q), .out(multiplexer_2_out), .sel(nor_9_out));  // open: en
  not not_6 (not_6_out, nor_9_out);
  Multiplexer multiplexer_3 (.in0(d_ff_11_qn), .in1(d_ff_11_q), .out(multiplexer_3_out), .sel(nor_10_out));  // open: en
  not not_7 (not_7_out, nor_10_out);
  D_Flip_Flop d_ff_14 (.clk(nACLK), .D(multiplexer_1_out), .Qn(d_ff_14_qn));  // open: Q, preset, en, reset
  D_Flip_Flop d_ff_15 (.clk(nACLK), .D(multiplexer_2_out), .Qn(d_ff_15_qn));  // open: Q, preset, en, reset
  D_Flip_Flop d_ff_16 (.clk(nACLK), .D(multiplexer_3_out), .Qn(d_ff_16_qn));  // open: Q, preset, en, reset
  nor nor_9 (nor_9_out, d_ff_9_q, not_5_out);
  nor nor_10 (nor_10_out, d_ff_10_q, not_6_out);
  nor nor_11 (nor_11_out, d_ff_11_q, not_7_out);
  nor nor_12 (ADDOUT, nor_3_out, d_ff_8_qn, NOSQA, SWCTRL, d_ff_17_qn, SWEEP, nLFO2);
  D_Flip_Flop d_ff_17 (.clk(nACLK), .D(nor_11_out), .Qn(d_ff_17_qn));  // open: Q, preset, en, reset
  D_Flip_Flop d_ff_18 (.clk(nACLK), .D(nor_11_out), .Q(d_ff_18_q));  // open: Qn, preset, en, reset

  assign SWEEP_2 = SWEEP;

  // Notes on the sheet:
  //   SR0
  //   SR1
  //   SR2
  //   DEC/INC
  //   P0
  //   P1
  //   P2
  //   SWDIS
  //   SWEEPRELOAD
  //   NOR2
  //   NOR1
  //   NOR7
  //   NORFF1
  //   RS1
  //   NORFF2
  //   NOR3
  //   NOR6
  //   INV1
  //   NOR5
  //   DL1
  //   DL2
  //   DL3
  //   NOR4
endmodule

// DIVIDER
module SQUARE_DIVIDER (
  input  nACLK,
  input  ACLK,
  input  W4000,
  input  W4003,
  input  RES,
  input  PL0,
  input  PL1,
  input  PL2,
  input  PL3,
  input  PL4,
  input  PL5,
  input  PL6,
  input  PL7,
  input  PL8,
  input  PL9,
  input  PL10,
  input  D6,
  input  D7,
  output FLOAD,
  output SQOUT
);

  wire and_1_out, and_2_out, and_3_out, and_4_out, and_5_out, and_6_out, and_7_out, and_8_out, and_9_out,
       and_10_out, and_11_out, and_12_out, and_13_out, and_14_out, and_15_out, and_16_out, and_17_out,
       and_18_out, and_19_out, and_20_out, and_21_out, and_22_out, and_23_out, d_ff_1_q, d_ff_1_qn, d_ff_2_q,
       d_ff_2_qn, d_ff_3_q, d_ff_3_qn, d_ff_4_q, d_ff_4_qn, d_ff_5_q, d_ff_5_qn, d_ff_6_q, d_ff_6_qn,
       d_ff_7_q, d_ff_7_qn, d_ff_8_q, d_ff_8_qn, d_ff_9_q, d_ff_9_qn, d_ff_10_q, d_ff_10_qn, d_ff_11_q,
       d_ff_11_qn, d_ff_12_q, d_ff_12_qn, d_ff_13_q, d_ff_13_qn, d_ff_14_q, d_ff_14_qn, d_ff_17_qn,
       d_ff_18_qn, d_ff_19_qn, d_ff_20_qn, d_ff_21_qn, d_ff_22_qn, d_ff_23_qn, d_ff_24_qn, d_ff_25_qn,
       d_ff_26_qn, d_ff_27_qn, d_ff_28_qn, d_ff_29_qn, d_ff_30_qn, d_ff_31_qn, multiplexer_1_out,
       multiplexer_2_out, multiplexer_3_out, multiplexer_4_out, multiplexer_5_out, multiplexer_6_out,
       multiplexer_7_out, multiplexer_8_out, multiplexer_9_out, multiplexer_10_out, multiplexer_11_out,
       multiplexer_12_out, multiplexer_13_out, multiplexer_14_out, nand_1_out, nor_2_out, nor_3_out,
       nor_4_out, nor_5_out, nor_6_out, nor_7_out, nor_8_out, nor_9_out, nor_10_out, nor_11_out, nor_12_out,
       nor_13_out, nor_14_out, nor_15_out, nor_16_out, not_1_out, not_2_out, not_3_out, not_4_out, not_5_out,
       not_6_out, not_7_out, not_8_out, not_9_out, not_10_out, not_11_out, not_12_out, not_13_out,
       not_14_out, not_15_out, not_16_out, not_17_out, not_18_out, not_19_out, not_20_out, not_21_out,
       not_22_out, not_23_out, not_24_out, not_25_out, not_26_out, not_27_out, or_1_out, or_2_out, or_3_out,
       or_4_out, or_5_out, or_6_out, or_7_out, or_8_out, or_9_out, or_10_out, or_11_out, or_12_out,
       or_13_out, or_14_out;
  wire [1:0] d_ff_15_q;
  wire [13:0] counter_1_q, register_1_q;

  Counter #(.width(14), .max('h3fff)) counter_1 (
    .Q(counter_1_q), .clk(nor_2_out), .clr(FLOAD));  // open: load, D, count, carry
  not not_1 (not_1_out, PL0);
  not not_2 (not_2_out, PL1);
  not not_3 (not_3_out, PL2);
  not not_4 (not_4_out, PL3);
  not not_5 (not_5_out, PL4);
  not not_6 (not_6_out, PL5);
  not not_7 (not_7_out, PL6);
  not not_8 (not_8_out, PL7);
  not not_9 (not_9_out, PL8);
  not not_10 (not_10_out, PL9);
  not not_11 (not_11_out, PL10);
  Register #(.width(14)) register_1 (.D(counter_1_q), .Q(register_1_q), .clk(FLOAD));  // open: en, clr
  D_Flip_Flop d_ff_1 (
    .clk(nor_2_out), .D(d_ff_17_qn), .Q(d_ff_1_q), .Qn(d_ff_1_qn), .preset(and_1_out), .reset(or_1_out));  // open: en
  and and_1 (and_1_out, FLOAD, PL0);
  and and_2 (and_2_out, FLOAD, not_1_out);
  or or_1 (or_1_out, and_2_out, RES);
  D_Flip_Flop d_ff_2 (
    .clk(nor_2_out), .D(d_ff_18_qn), .Q(d_ff_2_q), .Qn(d_ff_2_qn), .preset(and_3_out), .reset(or_2_out));  // open: en
  and and_3 (and_3_out, FLOAD, PL1);
  and and_4 (and_4_out, FLOAD, not_2_out);
  or or_2 (or_2_out, and_4_out, RES);
  D_Flip_Flop d_ff_3 (
    .clk(nor_2_out), .D(d_ff_19_qn), .Q(d_ff_3_q), .Qn(d_ff_3_qn), .preset(and_5_out), .reset(or_3_out));  // open: en
  and and_5 (and_5_out, FLOAD, PL2);
  and and_6 (and_6_out, FLOAD, not_3_out);
  or or_3 (or_3_out, and_6_out, RES);
  D_Flip_Flop d_ff_4 (
    .clk(nor_2_out), .D(d_ff_20_qn), .Q(d_ff_4_q), .Qn(d_ff_4_qn), .preset(and_7_out), .reset(or_4_out));  // open: en
  and and_7 (and_7_out, FLOAD, PL3);
  and and_8 (and_8_out, FLOAD, not_4_out);
  or or_4 (or_4_out, and_8_out, RES);
  D_Flip_Flop d_ff_5 (
    .clk(nor_2_out), .D(d_ff_21_qn), .Q(d_ff_5_q), .Qn(d_ff_5_qn), .preset(and_9_out), .reset(or_5_out));  // open: en
  and and_9 (and_9_out, FLOAD, PL4);
  and and_10 (and_10_out, FLOAD, not_5_out);
  or or_5 (or_5_out, and_10_out, RES);
  D_Flip_Flop d_ff_6 (
    .clk(nor_2_out), .D(d_ff_22_qn), .Q(d_ff_6_q), .Qn(d_ff_6_qn), .preset(and_11_out), .reset(or_6_out));  // open: en
  and and_11 (and_11_out, FLOAD, PL5);
  and and_12 (and_12_out, FLOAD, not_6_out);
  or or_6 (or_6_out, and_12_out, RES);
  D_Flip_Flop d_ff_7 (
    .clk(nor_2_out), .D(d_ff_23_qn), .Q(d_ff_7_q), .Qn(d_ff_7_qn), .preset(and_13_out), .reset(or_7_out));  // open: en
  and and_13 (and_13_out, FLOAD, PL6);
  and and_14 (and_14_out, FLOAD, not_7_out);
  or or_7 (or_7_out, and_14_out, RES);
  D_Flip_Flop d_ff_8 (
    .clk(nor_2_out), .D(d_ff_24_qn), .Q(d_ff_8_q), .Qn(d_ff_8_qn), .preset(and_15_out), .reset(or_8_out));  // open: en
  and and_15 (and_15_out, FLOAD, PL7);
  and and_16 (and_16_out, FLOAD, not_8_out);
  or or_8 (or_8_out, and_16_out, RES);
  D_Flip_Flop d_ff_9 (
    .clk(nor_2_out), .D(d_ff_25_qn), .Q(d_ff_9_q), .Qn(d_ff_9_qn), .preset(and_17_out), .reset(or_9_out));  // open: en
  and and_17 (and_17_out, FLOAD, PL8);
  and and_18 (and_18_out, FLOAD, not_9_out);
  or or_9 (or_9_out, and_18_out, RES);
  D_Flip_Flop d_ff_10 (
    .clk(nor_2_out), .D(d_ff_26_qn), .Q(d_ff_10_q), .Qn(d_ff_10_qn), .preset(and_19_out), .reset(or_10_out));  // open: en
  and and_19 (and_19_out, FLOAD, PL9);
  and and_20 (and_20_out, FLOAD, not_10_out);
  or or_10 (or_10_out, and_20_out, RES);
  D_Flip_Flop d_ff_11 (
    .clk(nor_2_out), .D(d_ff_27_qn), .Q(d_ff_11_q), .Qn(d_ff_11_qn), .preset(and_21_out), .reset(or_11_out));  // open: en
  and and_21 (and_21_out, FLOAD, PL10);
  and and_22 (and_22_out, FLOAD, not_11_out);
  or or_11 (or_11_out, and_22_out, RES);
  // Probe on register_1_q
  D_Flip_Flop d_ff_12 (
    .clk(FLOAD), .D(d_ff_28_qn), .Q(d_ff_12_q), .Qn(d_ff_12_qn), .reset(or_12_out));  // open: preset, en
  or or_12 (or_12_out, W4003, RES);
  D_Flip_Flop d_ff_13 (
    .clk(FLOAD), .D(d_ff_29_qn), .Q(d_ff_13_q), .Qn(d_ff_13_qn), .reset(or_13_out));  // open: preset, en
  or or_13 (or_13_out, W4003, RES);
  D_Flip_Flop d_ff_14 (
    .clk(FLOAD), .D(d_ff_30_qn), .Q(d_ff_14_q), .Qn(d_ff_14_qn), .reset(or_14_out));  // open: preset, en
  or or_14 (or_14_out, W4003, RES);
  D_Flip_Flop #(.trigger("high")) d_ff_15 (.clk(and_23_out), .D(D6), .Q(d_ff_15_q[0]));  // open: Qn, preset, en, reset
  and and_23 (and_23_out, ACLK, W4000);
  D_Flip_Flop #(.trigger("high")) d_ff_16 (.clk(and_23_out), .D(D7), .Q(d_ff_15_q[1]));  // open: Qn, preset, en, reset
  Multiplexer multiplexer_1 (.in0(d_ff_1_qn), .in1(d_ff_1_q), .out(multiplexer_1_out), .sel(1'b1));  // open: en
  Multiplexer multiplexer_2 (.in0(d_ff_2_qn), .in1(d_ff_2_q), .out(multiplexer_2_out), .sel(nor_3_out));  // open: en
  Multiplexer multiplexer_3 (.in0(d_ff_3_qn), .in1(d_ff_3_q), .out(multiplexer_3_out), .sel(nor_4_out));  // open: en
  Multiplexer multiplexer_4 (.in0(d_ff_4_qn), .in1(d_ff_4_q), .out(multiplexer_4_out), .sel(nor_5_out));  // open: en
  Multiplexer multiplexer_5 (.in0(d_ff_5_qn), .in1(d_ff_5_q), .out(multiplexer_5_out), .sel(nor_6_out));  // open: en
  Multiplexer multiplexer_6 (.in0(d_ff_6_qn), .in1(d_ff_6_q), .out(multiplexer_6_out), .sel(nor_7_out));  // open: en
  Multiplexer multiplexer_7 (.in0(d_ff_7_qn), .in1(d_ff_7_q), .out(multiplexer_7_out), .sel(nor_8_out));  // open: en
  Multiplexer multiplexer_8 (.in0(d_ff_8_qn), .in1(d_ff_8_q), .out(multiplexer_8_out), .sel(nor_9_out));  // open: en
  Multiplexer multiplexer_9 (.in0(d_ff_9_qn), .in1(d_ff_9_q), .out(multiplexer_9_out), .sel(nor_10_out));  // open: en
  Multiplexer multiplexer_10 (
    .in0(d_ff_10_qn), .in1(d_ff_10_q), .out(multiplexer_10_out), .sel(nor_11_out));  // open: en
  Multiplexer multiplexer_11 (
    .in0(d_ff_11_qn), .in1(d_ff_11_q), .out(multiplexer_11_out), .sel(nor_12_out));  // open: en
  nor nor_1 (FLOAD, d_ff_31_qn, nACLK);
  nor nor_2 (nor_2_out, nACLK, not_23_out);
  Multiplexer multiplexer_12 (
    .in0(d_ff_12_qn), .in1(d_ff_12_q), .out(multiplexer_12_out), .sel(nor_13_out));  // open: en
  Multiplexer multiplexer_13 (
    .in0(d_ff_13_qn), .in1(d_ff_13_q), .out(multiplexer_13_out), .sel(nor_14_out));  // open: en
  Multiplexer multiplexer_14 (
    .in0(d_ff_14_qn), .in1(d_ff_14_q), .out(multiplexer_14_out), .sel(nor_15_out));  // open: en
  D_Flip_Flop #(.trigger("high")) d_ff_17 (
    .clk(nACLK), .D(multiplexer_1_out), .Qn(d_ff_17_qn));  // open: Q, preset, en, reset
  not not_12 (not_12_out, 1'b1);
  D_Flip_Flop #(.trigger("high")) d_ff_18 (
    .clk(nACLK), .D(multiplexer_2_out), .Qn(d_ff_18_qn));  // open: Q, preset, en, reset
  not not_13 (not_13_out, nor_3_out);
  D_Flip_Flop #(.trigger("high")) d_ff_19 (
    .clk(nACLK), .D(multiplexer_3_out), .Qn(d_ff_19_qn));  // open: Q, preset, en, reset
  not not_14 (not_14_out, nor_4_out);
  D_Flip_Flop #(.trigger("high")) d_ff_20 (
    .clk(nACLK), .D(multiplexer_4_out), .Qn(d_ff_20_qn));  // open: Q, preset, en, reset
  not not_15 (not_15_out, nor_5_out);
  D_Flip_Flop #(.trigger("high")) d_ff_21 (
    .clk(nACLK), .D(multiplexer_5_out), .Qn(d_ff_21_qn));  // open: Q, preset, en, reset
  not not_16 (not_16_out, nor_6_out);
  D_Flip_Flop #(.trigger("high")) d_ff_22 (
    .clk(nACLK), .D(multiplexer_6_out), .Qn(d_ff_22_qn));  // open: Q, preset, en, reset
  not not_17 (not_17_out, nor_7_out);
  D_Flip_Flop #(.trigger("high")) d_ff_23 (
    .clk(nACLK), .D(multiplexer_7_out), .Qn(d_ff_23_qn));  // open: Q, preset, en, reset
  not not_18 (not_18_out, nor_8_out);
  D_Flip_Flop #(.trigger("high")) d_ff_24 (
    .clk(nACLK), .D(multiplexer_8_out), .Qn(d_ff_24_qn));  // open: Q, preset, en, reset
  not not_19 (not_19_out, nor_9_out);
  D_Flip_Flop #(.trigger("high")) d_ff_25 (
    .clk(nACLK), .D(multiplexer_9_out), .Qn(d_ff_25_qn));  // open: Q, preset, en, reset
  not not_20 (not_20_out, nor_10_out);
  D_Flip_Flop #(.trigger("high")) d_ff_26 (
    .clk(nACLK), .D(multiplexer_10_out), .Qn(d_ff_26_qn));  // open: Q, preset, en, reset
  not not_21 (not_21_out, nor_11_out);
  D_Flip_Flop #(.trigger("high")) d_ff_27 (
    .clk(nACLK), .D(multiplexer_11_out), .Qn(d_ff_27_qn));  // open: Q, preset, en, reset
  not not_22 (not_22_out, nor_12_out);
  not not_23 (not_23_out, d_ff_31_qn);
  D_Flip_Flop d_ff_28 (.clk(nACLK), .D(multiplexer_12_out), .Qn(d_ff_28_qn));  // open: Q, preset, en, reset
  not not_24 (not_24_out, nor_13_out);
  D_Flip_Flop d_ff_29 (.clk(nACLK), .D(multiplexer_13_out), .Qn(d_ff_29_qn));  // open: Q, preset, en, reset
  not not_25 (not_25_out, nor_14_out);
  D_Flip_Flop d_ff_30 (.clk(nACLK), .D(multiplexer_14_out), .Qn(d_ff_30_qn));  // open: Q, preset, en, reset
  nor nor_3 (nor_3_out, d_ff_1_q, not_12_out);
  nor nor_4 (nor_4_out, d_ff_2_q, not_13_out);
  nor nor_5 (nor_5_out, d_ff_3_q, not_14_out);
  nor nor_6 (nor_6_out, d_ff_4_q, not_15_out);
  nor nor_7 (nor_7_out, d_ff_5_q, not_16_out);
  nor nor_8 (nor_8_out, d_ff_6_q, not_17_out);
  nor nor_9 (nor_9_out, d_ff_7_q, not_18_out);
  nor nor_10 (nor_10_out, d_ff_8_q, not_19_out);
  nor nor_11 (nor_11_out, d_ff_9_q, not_20_out);
  nor nor_12 (nor_12_out, d_ff_10_q, not_21_out);
  nor nor_13 (nor_13_out, d_ff_11_q, not_22_out);
  nor nor_14 (nor_14_out, d_ff_12_q, not_24_out);
  nor nor_15 (nor_15_out, d_ff_13_q, not_25_out);
  not not_26 (not_26_out, d_ff_12_q);
  D_Flip_Flop d_ff_31 (.clk(nACLK), .D(nor_13_out), .Qn(d_ff_31_qn));  // open: Q, preset, en, reset
  nor nor_16 (nor_16_out, not_26_out, nand_1_out);
  not not_27 (not_27_out, nand_1_out);
  nand nand_1 (nand_1_out, d_ff_13_q, d_ff_14_q);
  Multiplexer #(.select(2)) multiplexer_15 (
    .in0(nor_16_out), .in1(not_27_out), .in2(d_ff_14_q), .in3(nand_1_out), .out(SQOUT), .sel(d_ff_15_q));  // open: en

  // Notes on the sheet:
  //   FLOAD
  //   NOR8
  //   STEP
  //   INV2
  //   DL4
  //   INV3
  //   NOR10
  //   INV4
  //   NAND1
  //   50%
  //   12.5%
  //   25%
  //   75%
endmodule

// ENVELOPE GENERATOR
module SQUARE_ENVELOPE_GENERATOR (
  input  nACLK,
  input  ACLK,
  input  W4000,
  input  W4003,
  input  D0,
  input  D1,
  input  D2,
  input  D3,
  input  D4,
  input  D5,
  input  nLFO1,
  input  RES,
  output VOL0,
  output VOL1,
  output VOL2,
  output VOL3,
  output ENVDIS,
  output Env0,
  output Env1,
  output Env2,
  output Env3
);

  wire and_1_out, and_2_out, and_3_out, and_4_out, and_5_out, and_6_out, and_7_out, and_8_out, and_9_out,
       and_10_out, and_11_out, and_12_out, and_13_out, and_14_out, and_15_out, and_16_out, and_17_out,
       d_ff_6_qn, d_ff_7_qn, d_ff_8_q, d_ff_9_q, d_ff_10_q, d_ff_11_q, d_ff_12_q, d_ff_12_qn, d_ff_13_q,
       d_ff_13_qn, d_ff_14_q, d_ff_14_qn, d_ff_15_q, d_ff_15_qn, d_ff_16_q, d_ff_17_qn, d_ff_18_qn,
       d_ff_19_qn, d_ff_20_qn, d_ff_21_qn, d_ff_22_qn, d_ff_23_qn, d_ff_24_qn, d_ff_25_qn, d_ff_26_qn,
       d_ff_27_qn, d_ff_28_qn, multiplexer_1_out, multiplexer_2_out, multiplexer_3_out, multiplexer_4_out,
       multiplexer_5_out, multiplexer_6_out, multiplexer_7_out, multiplexer_8_out, nand_1_out, nor_1_out,
       nor_2_out, nor_3_out, nor_4_out, nor_5_out, nor_6_out, nor_7_out, nor_8_out, nor_9_out, nor_10_out,
       nor_11_out, nor_12_out, nor_13_out, nor_14_out, nor_15_out, nor_16_out, nor_17_out, not_1_out,
       not_2_out, not_3_out, not_4_out, not_5_out, not_6_out, not_7_out, not_8_out, not_9_out, not_10_out,
       not_11_out, not_12_out, not_13_out, not_14_out, not_15_out, not_16_out, not_17_out, not_18_out,
       or_1_out, or_2_out, or_3_out, or_4_out, or_5_out, or_6_out, or_7_out, or_8_out;

  and and_1 (and_1_out, ACLK, W4000);
  D_Flip_Flop #(.trigger("high")) d_ff_1 (.clk(and_1_out), .D(D0), .Q(VOL0));  // open: Qn, preset, en, reset
  D_Flip_Flop #(.trigger("high")) d_ff_2 (.clk(and_1_out), .D(D1), .Q(VOL1));  // open: Qn, preset, en, reset
  D_Flip_Flop #(.trigger("high")) d_ff_3 (.clk(and_1_out), .D(D2), .Q(VOL2));  // open: Qn, preset, en, reset
  D_Flip_Flop #(.trigger("high")) d_ff_4 (.clk(and_1_out), .D(D3), .Q(VOL3));  // open: Qn, preset, en, reset
  D_Flip_Flop #(.trigger("high")) d_ff_5 (.clk(and_1_out), .D(D4), .Q(ENVDIS));  // open: Qn, preset, en, reset
  D_Flip_Flop #(.trigger("high")) d_ff_6 (.clk(and_1_out), .D(D5), .Qn(d_ff_6_qn));  // open: Q, preset, en, reset
  nor nor_1 (nor_1_out, nor_13_out, nor_2_out);
  not not_1 (not_1_out, VOL0);
  not not_2 (not_2_out, VOL1);
  not not_3 (not_3_out, VOL2);
  not not_4 (not_4_out, VOL3);
  D_Flip_Flop d_ff_7 (.clk(nACLK), .D(nor_1_out), .Qn(d_ff_7_qn));  // open: Q, preset, en, reset
  D_Flip_Flop d_ff_8 (.clk(nACLK), .D(nor_1_out), .Q(d_ff_8_q));  // open: Qn, preset, en, reset
  not not_5 (not_5_out, nand_1_out);
  not not_6 (not_6_out, nand_1_out);
  not not_7 (not_7_out, nand_1_out);
  not not_8 (not_8_out, nand_1_out);
  D_Flip_Flop d_ff_9 (.clk(nACLK), .D(nor_17_out), .Q(d_ff_9_q));  // open: Qn, preset, en, reset
  D_Flip_Flop d_ff_10 (.clk(nACLK), .D(nor_17_out), .Q(d_ff_10_q));  // open: Qn, preset, en, reset
  D_Flip_Flop d_ff_11 (.clk(nACLK), .D(nor_2_out), .Q(d_ff_11_q));  // open: Qn, preset, en, reset
  and and_2 (and_2_out, VOL0, nor_5_out);
  and and_3 (and_3_out, not_1_out, nor_5_out);
  and and_4 (and_4_out, VOL1, nor_5_out);
  and and_5 (and_5_out, not_2_out, nor_5_out);
  and and_6 (and_6_out, VOL2, nor_5_out);
  and and_7 (and_7_out, not_3_out, nor_5_out);
  and and_8 (and_8_out, VOL3, nor_5_out);
  and and_9 (and_9_out, not_4_out, nor_5_out);
  nor nor_2 (nor_2_out, nor_7_out, nor_3_out);
  nor nor_3 (nor_3_out, nor_2_out, W4003);
  nor nor_4 (nor_4_out, d_ff_7_qn, nLFO1);
  nor nor_5 (nor_5_out, d_ff_8_q, nLFO1);
  and and_10 (and_10_out, nand_1_out, nor_9_out);
  and and_11 (and_11_out, not_5_out, nor_9_out);
  and and_12 (and_12_out, nand_1_out, nor_9_out);
  and and_13 (and_13_out, not_6_out, nor_9_out);
  and and_14 (and_14_out, nand_1_out, nor_9_out);
  and and_15 (and_15_out, not_7_out, nor_9_out);
  and and_16 (and_16_out, nand_1_out, nor_9_out);
  and and_17 (and_17_out, not_8_out, nor_9_out);
  nand nand_1 (nand_1_out, d_ff_9_q, d_ff_6_qn);
  nor nor_6 (nor_6_out, d_ff_10_q, d_ff_11_q);
  D_Flip_Flop d_ff_12 (
    .clk(nor_4_out), .D(d_ff_21_qn), .Q(d_ff_12_q), .Qn(d_ff_12_qn), .preset(and_2_out), .reset(or_1_out));  // open: en
  or or_1 (or_1_out, and_3_out, RES);
  D_Flip_Flop d_ff_13 (
    .clk(nor_4_out), .D(d_ff_22_qn), .Q(d_ff_13_q), .Qn(d_ff_13_qn), .preset(and_4_out), .reset(or_2_out));  // open: en
  or or_2 (or_2_out, and_5_out, RES);
  D_Flip_Flop d_ff_14 (
    .clk(nor_4_out), .D(d_ff_23_qn), .Q(d_ff_14_q), .Qn(d_ff_14_qn), .preset(and_6_out), .reset(or_3_out));  // open: en
  or or_3 (or_3_out, and_7_out, RES);
  D_Flip_Flop d_ff_15 (
    .clk(nor_4_out), .D(d_ff_24_qn), .Q(d_ff_15_q), .Qn(d_ff_15_qn), .preset(and_8_out), .reset(or_4_out));  // open: en
  or or_4 (or_4_out, and_9_out, RES);
  D_Flip_Flop d_ff_16 (.clk(nACLK), .D(nor_3_out), .Q(d_ff_16_q));  // open: Qn, preset, en, reset
  D_Flip_Flop d_ff_17 (
    .clk(nor_8_out), .D(d_ff_25_qn), .Q(Env0), .Qn(d_ff_17_qn), .preset(and_10_out), .reset(or_5_out));  // open: en
  or or_5 (or_5_out, and_11_out, RES);
  D_Flip_Flop d_ff_18 (
    .clk(nor_8_out), .D(d_ff_26_qn), .Q(Env1), .Qn(d_ff_18_qn), .preset(and_12_out), .reset(or_6_out));  // open: en
  or or_6 (or_6_out, and_13_out, RES);
  D_Flip_Flop d_ff_19 (
    .clk(nor_8_out), .D(d_ff_27_qn), .Q(Env2), .Qn(d_ff_19_qn), .preset(and_14_out), .reset(or_7_out));  // open: en
  or or_7 (or_7_out, and_15_out, RES);
  D_Flip_Flop d_ff_20 (
    .clk(nor_8_out), .D(d_ff_28_qn), .Q(Env3), .Qn(d_ff_20_qn), .preset(and_16_out), .reset(or_8_out));  // open: en
  or or_8 (or_8_out, and_17_out, RES);
  not not_9 (not_9_out, nor_5_out);
  not not_10 (not_10_out, nor_6_out);
  Multiplexer multiplexer_1 (.in0(d_ff_12_qn), .in1(d_ff_12_q), .out(multiplexer_1_out), .sel(1'b1));  // open: en
  not not_11 (not_11_out, 1'b1);
  Multiplexer multiplexer_2 (.in0(d_ff_13_qn), .in1(d_ff_13_q), .out(multiplexer_2_out), .sel(nor_10_out));  // open: en
  not not_12 (not_12_out, nor_10_out);
  Multiplexer multiplexer_3 (.in0(d_ff_14_qn), .in1(d_ff_14_q), .out(multiplexer_3_out), .sel(nor_11_out));  // open: en
  not not_13 (not_13_out, nor_11_out);
  Multiplexer multiplexer_4 (.in0(d_ff_15_qn), .in1(d_ff_15_q), .out(multiplexer_4_out), .sel(nor_12_out));  // open: en
  not not_14 (not_14_out, nor_12_out);
  nor nor_7 (nor_7_out, d_ff_16_q, nLFO1);
  Multiplexer multiplexer_5 (.in0(d_ff_17_qn), .in1(Env0), .out(multiplexer_5_out), .sel(1'b1));  // open: en
  not not_15 (not_15_out, 1'b1);
  Multiplexer multiplexer_6 (.in0(d_ff_18_qn), .in1(Env1), .out(multiplexer_6_out), .sel(nor_14_out));  // open: en
  not not_16 (not_16_out, nor_14_out);
  Multiplexer multiplexer_7 (.in0(d_ff_19_qn), .in1(Env2), .out(multiplexer_7_out), .sel(nor_15_out));  // open: en
  not not_17 (not_17_out, nor_15_out);
  Multiplexer multiplexer_8 (.in0(d_ff_20_qn), .in1(Env3), .out(multiplexer_8_out), .sel(nor_16_out));  // open: en
  not not_18 (not_18_out, nor_16_out);
  nor nor_8 (nor_8_out, not_9_out, not_10_out);
  nor nor_9 (nor_9_out, not_9_out, nor_6_out);
  D_Flip_Flop d_ff_21 (.clk(nACLK), .D(multiplexer_1_out), .Qn(d_ff_21_qn));  // open: Q, preset, en, reset
  D_Flip_Flop d_ff_22 (.clk(nACLK), .D(multiplexer_2_out), .Qn(d_ff_22_qn));  // open: Q, preset, en, reset
  D_Flip_Flop d_ff_23 (.clk(nACLK), .D(multiplexer_3_out), .Qn(d_ff_23_qn));  // open: Q, preset, en, reset
  D_Flip_Flop d_ff_24 (.clk(nACLK), .D(multiplexer_4_out), .Qn(d_ff_24_qn));  // open: Q, preset, en, reset
  D_Flip_Flop d_ff_25 (.clk(nACLK), .D(multiplexer_5_out), .Qn(d_ff_25_qn));  // open: Q, preset, en, reset
  D_Flip_Flop d_ff_26 (.clk(nACLK), .D(multiplexer_6_out), .Qn(d_ff_26_qn));  // open: Q, preset, en, reset
  D_Flip_Flop d_ff_27 (.clk(nACLK), .D(multiplexer_7_out), .Qn(d_ff_27_qn));  // open: Q, preset, en, reset
  D_Flip_Flop d_ff_28 (.clk(nACLK), .D(multiplexer_8_out), .Qn(d_ff_28_qn));  // open: Q, preset, en, reset
  nor nor_10 (nor_10_out, d_ff_12_q, not_11_out);
  nor nor_11 (nor_11_out, d_ff_13_q, not_12_out);
  nor nor_12 (nor_12_out, d_ff_14_q, not_13_out);
  nor nor_13 (nor_13_out, d_ff_15_q, not_14_out);
  nor nor_14 (nor_14_out, Env0, not_15_out);
  nor nor_15 (nor_15_out, Env1, not_16_out);
  nor nor_16 (nor_16_out, Env2, not_17_out);
  nor nor_17 (nor_17_out, Env3, nor_2_out, not_18_out);

  // Notes on the sheet:
  //   ENDIS
  //   SQA/LC
  //   NOR17
  //   RS1
  //   NORFF2
  //   DL10
  //   DL11
  //   DL7
  //   DL8
  //   DL9
  //   NORFF1
  //   NOR16
  //   NOR15
  //   LOAD
  //   NAND2
  //   NOR18
  //   RELOAD
  //   DL6
  //   RSTEP
  //   INV6
  //   INV7
  //   NOR12
  //   ESTEP
  //   NOR19
  //   NOR14
  //   ERES
endmodule

// SQUARE CHANNEL 0
module SQUARE_CHANNEL_0 (
  input  ACLK,
  input  nACLK,
  input  W4000,
  input  W4001,
  input  W4002,
  input  W4003,
  input  D0,
  input  D1,
  input  D2,
  input  D3,
  input  D4,
  input  D5,
  input  D6,
  input  D7,
  input  NOSQA,
  input  RES,
  input  nLFO1,
  input  nLFO2,
  output SQA0,
  output SQA1,
  output SQ2,
  output SQA3
);

  wire d_ff_1_qn, multiplexer_1_out, multiplexer_2_out, multiplexer_3_out, multiplexer_4_out, nor_1_out,
       not_1_out, not_2_out, not_3_out, not_4_out, not_5_out, square_adder_1_ncout, square_adder_1_pl0,
       square_adder_1_pl1, square_adder_1_pl2, square_adder_1_pl3, square_adder_1_pl4, square_adder_1_pl5,
       square_adder_1_pl6, square_adder_1_pl7, square_adder_1_pl8, square_adder_1_pl9, square_adder_1_pl10,
       square_adder_1_sweep, square_divider_1_fload, square_divider_1_sqout,
       square_envelope_generator_1_env0, square_envelope_generator_1_env1, square_envelope_generator_1_env2,
       square_envelope_generator_1_env3, square_envelope_generator_1_envdis,
       square_envelope_generator_1_vol0, square_envelope_generator_1_vol1, square_envelope_generator_1_vol2,
       square_envelope_generator_1_vol3, square_sweep_control_1_addout, square_sweep_control_1_d_i,
       square_sweep_control_1_sr0, square_sweep_control_1_sr1, square_sweep_control_1_sr2,
       square_sweep_control_1_swctrl, square_sweep_control_1_sweep_2;

  SQUARE_ADDER square_adder_1 (
    .nACLK(nACLK), .ACLK(ACLK), .W4002(W4002), .W4003(W4003), .D0(D0), .D1(D1), .D2(D2), .D3(D3), .D4(D4),
    .D5(D5), .D6(D6), .D7(D7), .Dec_Inc(square_sweep_control_1_d_i), .SR0(square_sweep_control_1_sr0),
    .SR1(square_sweep_control_1_sr1), .SR2(square_sweep_control_1_sr2),
    .Addout(square_sweep_control_1_addout), .PL0(square_adder_1_pl0), .PL1(square_adder_1_pl1),
    .PL2(square_adder_1_pl2), .PL3(square_adder_1_pl3), .PL4(square_adder_1_pl4), .PL5(square_adder_1_pl5),
    .PL6(square_adder_1_pl6), .PL7(square_adder_1_pl7), .PL8(square_adder_1_pl8), .PL9(square_adder_1_pl9),
    .PL10(square_adder_1_pl10), .nCOUT(square_adder_1_ncout), .SWEEP(square_adder_1_sweep));
  SQUARE_SWEEP_CONTROL square_sweep_control_1 (
    .nACLK(nACLK), .ACLK(ACLK), .W4001(W4001), .D0(D0), .D1(D1), .D2(D2), .D3(D3), .D4(D4), .D5(D5), .D6(D6),
    .D7(D7), .nLFO2(nLFO2), .NOSQA(NOSQA), .nCOUT(square_adder_1_ncout), .SWEEP(square_adder_1_sweep),
    .RES(RES), .SR0(square_sweep_control_1_sr0), .SR1(square_sweep_control_1_sr1),
    .SR2(square_sweep_control_1_sr2), .D_I(square_sweep_control_1_d_i),
    .ADDOUT(square_sweep_control_1_addout), .SWEEP_2(square_sweep_control_1_sweep_2),
    .SWCTRL(square_sweep_control_1_swctrl));
  SQUARE_DIVIDER square_divider_1 (
    .nACLK(nACLK), .ACLK(ACLK), .W4000(W4000), .W4003(W4003), .RES(RES), .PL0(square_adder_1_pl0),
    .PL1(square_adder_1_pl1), .PL2(square_adder_1_pl2), .PL3(square_adder_1_pl3), .PL4(square_adder_1_pl4),
    .PL5(square_adder_1_pl5), .PL6(square_adder_1_pl6), .PL7(square_adder_1_pl7), .PL8(square_adder_1_pl8),
    .PL9(square_adder_1_pl9), .PL10(square_adder_1_pl10), .D6(D6), .D7(D7), .FLOAD(square_divider_1_fload),
    .SQOUT(square_divider_1_sqout));
  not not_1 (not_1_out, square_divider_1_sqout);
  nor nor_1 (nor_1_out, not_1_out, NOSQA, square_sweep_control_1_sweep_2, square_sweep_control_1_swctrl);
  D_Flip_Flop d_ff_1 (.clk(nACLK), .D(nor_1_out), .Qn(d_ff_1_qn));  // open: Q, preset, en, reset
  SQUARE_ENVELOPE_GENERATOR square_envelope_generator_1 (
    .nACLK(nACLK), .ACLK(ACLK), .W4000(W4000), .W4003(W4003), .D0(D0), .D1(D1), .D2(D2), .D3(D3), .D4(D4),
    .D5(D5), .nLFO1(nLFO1), .RES(RES), .VOL0(square_envelope_generator_1_vol0),
    .VOL1(square_envelope_generator_1_vol1), .VOL2(square_envelope_generator_1_vol2),
    .VOL3(square_envelope_generator_1_vol3), .ENVDIS(square_envelope_generator_1_envdis),
    .Env0(square_envelope_generator_1_env0), .Env1(square_envelope_generator_1_env1),
    .Env2(square_envelope_generator_1_env2), .Env3(square_envelope_generator_1_env3));
  nor nor_2 (SQA0, not_2_out, d_ff_1_qn);
  nor nor_3 (SQA1, not_3_out, d_ff_1_qn);
  nor nor_4 (SQ2, not_4_out, d_ff_1_qn);
  nor nor_5 (SQA3, not_5_out, d_ff_1_qn);
  not not_2 (not_2_out, multiplexer_1_out);
  Multiplexer #(.enable("false")) multiplexer_1 (
    .in0(square_envelope_generator_1_env0), .in1(square_envelope_generator_1_vol0), .out(multiplexer_1_out),
    .sel(square_envelope_generator_1_envdis));
  Multiplexer #(.enable("false")) multiplexer_2 (
    .in0(square_envelope_generator_1_env1), .in1(square_envelope_generator_1_vol1), .out(multiplexer_2_out),
    .sel(square_envelope_generator_1_envdis));
  not not_3 (not_3_out, multiplexer_2_out);
  not not_4 (not_4_out, multiplexer_3_out);
  Multiplexer #(.enable("false")) multiplexer_3 (
    .in0(square_envelope_generator_1_env2), .in1(square_envelope_generator_1_vol2), .out(multiplexer_3_out),
    .sel(square_envelope_generator_1_envdis));
  Multiplexer #(.enable("false")) multiplexer_4 (
    .in0(square_envelope_generator_1_env3), .in1(square_envelope_generator_1_vol3), .out(multiplexer_4_out),
    .sel(square_envelope_generator_1_envdis));
  not not_5 (not_5_out, multiplexer_4_out);

  // Notes on the sheet:
  //   INV5
  //   DL5
endmodule

// TRIANGLE CHANNEL
module TRIANGLE_CHANNEL (
  input  PHI1,
  input  PHI2,
  input  ACLK,
  input  nACLK,
  input  W4008,
  input  W400A,
  input  W400B,
  input  D0,
  input  D1,
  input  D2,
  input  D3,
  input  D4,
  input  D5,
  input  D6,
  input  D7,
  input  nLFO1,
  input  RES,
  input  NOTRI,
  output TRI0,
  output TRI1,
  output TRI2,
  output TRI3,
  output TRI_LC
);

  wire nor_1_out, triangle_divider_1_fload, triangle_divider_1_fout, triangle_linear_counter_1_out;

  TRIANGLE_DIVIDER triangle_divider_1 (
    .nACLK(PHI1), .ACLK(PHI2), .W400A(W400A), .W400B(W400B), .RES(RES), .D0(D0), .D1(D1), .D2(D2), .D3(D3),
    .D4(D4), .D5(D5), .D6(D6), .D7(D7), .FLOAD(triangle_divider_1_fload), .FOUT(triangle_divider_1_fout));
  TRIANGLE_LINEAR_COUNTER triangle_linear_counter_1 (
    .nACLK(nACLK), .ACLK(ACLK), .W4008(W4008), .W400B(W400B), .nLFO1(nLFO1), .RES(RES), .D0(D0), .D1(D1),
    .D2(D2), .D3(D3), .D4(D4), .D5(D5), .OUT(triangle_linear_counter_1_out), .D6(D6), .D7(D7), .TRI_LC(TRI_LC));
  nor nor_1 (nor_1_out, PHI1, triangle_divider_1_fout, triangle_linear_counter_1_out, NOTRI);
  TRIANGLE_OUTPUT_COUNTER triangle_output_counter_1 (
    .PHI1(PHI1), .TSTEP(nor_1_out), .RES(RES), .TRI0(TRI0), .TRI1(TRI1), .TRI2(TRI2), .TRI3(TRI3));

  // Notes on the sheet:
  //   NOR3
endmodule

// TRIANGLE DIVIDER
module TRIANGLE_DIVIDER (
  input  nACLK,
  input  ACLK,
  input  W400A,
  input  W400B,
  input  RES,
  input  D0,
  input  D1,
  input  D2,
  input  D3,
  input  D4,
  input  D5,
  input  D6,
  input  D7,
  output FLOAD,
  output FOUT
);

  wire and_1_out, and_2_out, and_3_out, and_4_out, and_5_out, and_6_out, and_7_out, and_8_out, and_9_out,
       and_10_out, and_11_out, and_12_out, and_13_out, and_14_out, and_15_out, and_16_out, and_17_out,
       and_18_out, and_19_out, and_20_out, and_21_out, and_22_out, and_23_out, and_24_out, d_ff_1_q,
       d_ff_2_q, d_ff_3_q, d_ff_4_q, d_ff_5_q, d_ff_6_q, d_ff_7_q, d_ff_8_q, d_ff_9_q, d_ff_10_q, d_ff_11_q,
       d_ff_12_q, d_ff_12_qn, d_ff_13_q, d_ff_13_qn, d_ff_14_q, d_ff_14_qn, d_ff_15_q, d_ff_15_qn, d_ff_16_q,
       d_ff_16_qn, d_ff_17_q, d_ff_17_qn, d_ff_18_q, d_ff_18_qn, d_ff_19_q, d_ff_19_qn, d_ff_20_q,
       d_ff_20_qn, d_ff_21_q, d_ff_21_qn, d_ff_22_q, d_ff_22_qn, d_ff_23_qn, d_ff_24_qn, d_ff_25_qn,
       d_ff_26_qn, d_ff_27_qn, d_ff_28_qn, d_ff_29_qn, d_ff_30_qn, d_ff_31_qn, d_ff_32_qn, d_ff_33_qn,
       multiplexer_1_out, multiplexer_2_out, multiplexer_3_out, multiplexer_4_out, multiplexer_5_out,
       multiplexer_6_out, multiplexer_7_out, multiplexer_8_out, multiplexer_9_out, multiplexer_10_out,
       multiplexer_11_out, nor_1_out, nor_3_out, nor_4_out, nor_5_out, nor_6_out, nor_7_out, nor_8_out,
       nor_9_out, nor_10_out, nor_11_out, nor_12_out, nor_13_out, not_1_out, not_2_out, not_3_out, not_4_out,
       not_5_out, not_6_out, not_7_out, not_8_out, not_9_out, not_10_out, not_11_out, not_12_out, not_13_out,
       not_14_out, not_15_out, not_16_out, not_17_out, not_18_out, not_19_out, not_20_out, not_21_out,
       not_22_out, not_23_out, or_1_out, or_2_out, or_3_out, or_4_out, or_5_out, or_6_out, or_7_out,
       or_8_out, or_9_out, or_10_out, or_11_out;

  and and_1 (and_1_out, ACLK, W400A);
  and and_2 (and_2_out, ACLK, W400B);
  D_Flip_Flop #(.trigger("high")) d_ff_1 (.clk(and_1_out), .D(D0), .Q(d_ff_1_q));  // open: Qn, preset, en, reset
  D_Flip_Flop #(.trigger("high")) d_ff_2 (.clk(and_1_out), .D(D1), .Q(d_ff_2_q));  // open: Qn, preset, en, reset
  D_Flip_Flop #(.trigger("high")) d_ff_3 (.clk(and_1_out), .D(D2), .Q(d_ff_3_q));  // open: Qn, preset, en, reset
  D_Flip_Flop #(.trigger("high")) d_ff_4 (.clk(and_1_out), .D(D3), .Q(d_ff_4_q));  // open: Qn, preset, en, reset
  D_Flip_Flop #(.trigger("high")) d_ff_5 (.clk(and_1_out), .D(D4), .Q(d_ff_5_q));  // open: Qn, preset, en, reset
  D_Flip_Flop #(.trigger("high")) d_ff_6 (.clk(and_1_out), .D(D5), .Q(d_ff_6_q));  // open: Qn, preset, en, reset
  D_Flip_Flop #(.trigger("high")) d_ff_7 (.clk(and_1_out), .D(D6), .Q(d_ff_7_q));  // open: Qn, preset, en, reset
  D_Flip_Flop #(.trigger("high")) d_ff_8 (.clk(and_1_out), .D(D7), .Q(d_ff_8_q));  // open: Qn, preset, en, reset
  D_Flip_Flop #(.trigger("high")) d_ff_9 (.clk(and_2_out), .D(D0), .Q(d_ff_9_q));  // open: Qn, preset, en, reset
  D_Flip_Flop #(.trigger("high")) d_ff_10 (.clk(and_2_out), .D(D1), .Q(d_ff_10_q));  // open: Qn, preset, en, reset
  D_Flip_Flop #(.trigger("high")) d_ff_11 (.clk(and_2_out), .D(D2), .Q(d_ff_11_q));  // open: Qn, preset, en, reset
  not not_1 (not_1_out, d_ff_1_q);
  not not_2 (not_2_out, d_ff_2_q);
  not not_3 (not_3_out, d_ff_3_q);
  not not_4 (not_4_out, d_ff_4_q);
  not not_5 (not_5_out, d_ff_5_q);
  not not_6 (not_6_out, d_ff_6_q);
  not not_7 (not_7_out, d_ff_7_q);
  not not_8 (not_8_out, d_ff_8_q);
  not not_9 (not_9_out, d_ff_9_q);
  not not_10 (not_10_out, d_ff_10_q);
  not not_11 (not_11_out, d_ff_11_q);
  and and_3 (and_3_out, FLOAD, d_ff_1_q);
  and and_4 (and_4_out, FLOAD, not_1_out);
  and and_5 (and_5_out, FLOAD, d_ff_2_q);
  and and_6 (and_6_out, FLOAD, not_2_out);
  and and_7 (and_7_out, FLOAD, d_ff_3_q);
  and and_8 (and_8_out, FLOAD, not_3_out);
  and and_9 (and_9_out, FLOAD, d_ff_4_q);
  and and_10 (and_10_out, FLOAD, not_4_out);
  and and_11 (and_11_out, FLOAD, d_ff_5_q);
  and and_12 (and_12_out, FLOAD, not_5_out);
  and and_13 (and_13_out, FLOAD, d_ff_6_q);
  and and_14 (and_14_out, FLOAD, not_6_out);
  and and_15 (and_15_out, FLOAD, d_ff_7_q);
  and and_16 (and_16_out, FLOAD, not_7_out);
  and and_17 (and_17_out, FLOAD, d_ff_8_q);
  and and_18 (and_18_out, FLOAD, not_8_out);
  and and_19 (and_19_out, FLOAD, d_ff_9_q);
  and and_20 (and_20_out, FLOAD, not_9_out);
  and and_21 (and_21_out, FLOAD, d_ff_10_q);
  and and_22 (and_22_out, FLOAD, not_10_out);
  and and_23 (and_23_out, FLOAD, d_ff_11_q);
  and and_24 (and_24_out, FLOAD, not_11_out);
  D_Flip_Flop d_ff_12 (
    .clk(nor_1_out), .D(d_ff_23_qn), .Q(d_ff_12_q), .Qn(d_ff_12_qn), .preset(and_3_out), .reset(or_1_out));  // open: en
  or or_1 (or_1_out, and_4_out, RES);
  D_Flip_Flop d_ff_13 (
    .clk(nor_1_out), .D(d_ff_24_qn), .Q(d_ff_13_q), .Qn(d_ff_13_qn), .preset(and_5_out), .reset(or_2_out));  // open: en
  or or_2 (or_2_out, and_6_out, RES);
  D_Flip_Flop d_ff_14 (
    .clk(nor_1_out), .D(d_ff_25_qn), .Q(d_ff_14_q), .Qn(d_ff_14_qn), .preset(and_7_out), .reset(or_3_out));  // open: en
  or or_3 (or_3_out, and_8_out, RES);
  D_Flip_Flop d_ff_15 (
    .clk(nor_1_out), .D(d_ff_26_qn), .Q(d_ff_15_q), .Qn(d_ff_15_qn), .preset(and_9_out), .reset(or_4_out));  // open: en
  or or_4 (or_4_out, and_10_out, RES);
  D_Flip_Flop d_ff_16 (
    .clk(nor_1_out), .D(d_ff_27_qn), .Q(d_ff_16_q), .Qn(d_ff_16_qn), .preset(and_11_out), .reset(or_5_out));  // open: en
  or or_5 (or_5_out, and_12_out, RES);
  D_Flip_Flop d_ff_17 (
    .clk(nor_1_out), .D(d_ff_28_qn), .Q(d_ff_17_q), .Qn(d_ff_17_qn), .preset(and_13_out), .reset(or_6_out));  // open: en
  or or_6 (or_6_out, and_14_out, RES);
  D_Flip_Flop d_ff_18 (
    .clk(nor_1_out), .D(d_ff_29_qn), .Q(d_ff_18_q), .Qn(d_ff_18_qn), .preset(and_15_out), .reset(or_7_out));  // open: en
  or or_7 (or_7_out, and_16_out, RES);
  D_Flip_Flop d_ff_19 (
    .clk(nor_1_out), .D(d_ff_30_qn), .Q(d_ff_19_q), .Qn(d_ff_19_qn), .preset(and_17_out), .reset(or_8_out));  // open: en
  or or_8 (or_8_out, and_18_out, RES);
  D_Flip_Flop d_ff_20 (
    .clk(nor_1_out), .D(d_ff_31_qn), .Q(d_ff_20_q), .Qn(d_ff_20_qn), .preset(and_19_out), .reset(or_9_out));  // open: en
  or or_9 (or_9_out, and_20_out, RES);
  D_Flip_Flop d_ff_21 (
    .clk(nor_1_out), .D(d_ff_32_qn), .Q(d_ff_21_q), .Qn(d_ff_21_qn), .preset(and_21_out), .reset(or_10_out));  // open: en
  or or_10 (or_10_out, and_22_out, RES);
  D_Flip_Flop d_ff_22 (
    .clk(nor_1_out), .D(d_ff_33_qn), .Q(d_ff_22_q), .Qn(d_ff_22_qn), .preset(and_23_out), .reset(or_11_out));  // open: en
  or or_11 (or_11_out, and_24_out, RES);
  nor nor_1 (nor_1_out, not_23_out, nACLK);
  nor nor_2 (FLOAD, FOUT, nACLK);
  Multiplexer multiplexer_1 (.in0(d_ff_12_qn), .in1(d_ff_12_q), .out(multiplexer_1_out), .sel(1'b1));  // open: en
  Multiplexer multiplexer_2 (.in0(d_ff_13_qn), .in1(d_ff_13_q), .out(multiplexer_2_out), .sel(nor_3_out));  // open: en
  Multiplexer multiplexer_3 (.in0(d_ff_14_qn), .in1(d_ff_14_q), .out(multiplexer_3_out), .sel(nor_4_out));  // open: en
  Multiplexer multiplexer_4 (.in0(d_ff_15_qn), .in1(d_ff_15_q), .out(multiplexer_4_out), .sel(nor_5_out));  // open: en
  Multiplexer multiplexer_5 (.in0(d_ff_16_qn), .in1(d_ff_16_q), .out(multiplexer_5_out), .sel(nor_6_out));  // open: en
  Multiplexer multiplexer_6 (.in0(d_ff_17_qn), .in1(d_ff_17_q), .out(multiplexer_6_out), .sel(nor_7_out));  // open: en
  Multiplexer multiplexer_7 (.in0(d_ff_18_qn), .in1(d_ff_18_q), .out(multiplexer_7_out), .sel(nor_8_out));  // open: en
  Multiplexer multiplexer_8 (.in0(d_ff_19_qn), .in1(d_ff_19_q), .out(multiplexer_8_out), .sel(nor_9_out));  // open: en
  Multiplexer multiplexer_9 (.in0(d_ff_20_qn), .in1(d_ff_20_q), .out(multiplexer_9_out), .sel(nor_10_out));  // open: en
  Multiplexer multiplexer_10 (
    .in0(d_ff_21_qn), .in1(d_ff_21_q), .out(multiplexer_10_out), .sel(nor_11_out));  // open: en
  Multiplexer multiplexer_11 (
    .in0(d_ff_22_qn), .in1(d_ff_22_q), .out(multiplexer_11_out), .sel(nor_12_out));  // open: en
  D_Flip_Flop d_ff_23 (.clk(nACLK), .D(multiplexer_1_out), .Qn(d_ff_23_qn));  // open: Q, preset, en, reset
  not not_12 (not_12_out, 1'b1);
  D_Flip_Flop d_ff_24 (.clk(nACLK), .D(multiplexer_2_out), .Qn(d_ff_24_qn));  // open: Q, preset, en, reset
  not not_13 (not_13_out, nor_3_out);
  D_Flip_Flop d_ff_25 (.clk(nACLK), .D(multiplexer_3_out), .Qn(d_ff_25_qn));  // open: Q, preset, en, reset
  not not_14 (not_14_out, nor_4_out);
  D_Flip_Flop d_ff_26 (.clk(nACLK), .D(multiplexer_4_out), .Qn(d_ff_26_qn));  // open: Q, preset, en, reset
  not not_15 (not_15_out, nor_5_out);
  D_Flip_Flop d_ff_27 (.clk(nACLK), .D(multiplexer_5_out), .Qn(d_ff_27_qn));  // open: Q, preset, en, reset
  not not_16 (not_16_out, nor_6_out);
  D_Flip_Flop d_ff_28 (.clk(nACLK), .D(multiplexer_6_out), .Qn(d_ff_28_qn));  // open: Q, preset, en, reset
  not not_17 (not_17_out, nor_7_out);
  D_Flip_Flop d_ff_29 (.clk(nACLK), .D(multiplexer_7_out), .Qn(d_ff_29_qn));  // open: Q, preset, en, reset
  not not_18 (not_18_out, nor_8_out);
  D_Flip_Flop d_ff_30 (.clk(nACLK), .D(multiplexer_8_out), .Qn(d_ff_30_qn));  // open: Q, preset, en, reset
  not not_19 (not_19_out, nor_9_out);
  D_Flip_Flop d_ff_31 (.clk(nACLK), .D(multiplexer_9_out), .Qn(d_ff_31_qn));  // open: Q, preset, en, reset
  not not_20 (not_20_out, nor_10_out);
  D_Flip_Flop d_ff_32 (.clk(nACLK), .D(multiplexer_10_out), .Qn(d_ff_32_qn));  // open: Q, preset, en, reset
  not not_21 (not_21_out, nor_11_out);
  D_Flip_Flop d_ff_33 (.clk(nACLK), .D(multiplexer_11_out), .Qn(d_ff_33_qn));  // open: Q, preset, en, reset
  not not_22 (not_22_out, nor_12_out);
  nor nor_3 (nor_3_out, d_ff_12_q, not_12_out);
  nor nor_4 (nor_4_out, d_ff_13_q, not_13_out);
  nor nor_5 (nor_5_out, d_ff_14_q, not_14_out);
  nor nor_6 (nor_6_out, d_ff_15_q, not_15_out);
  nor nor_7 (nor_7_out, d_ff_16_q, not_16_out);
  nor nor_8 (nor_8_out, d_ff_17_q, not_17_out);
  nor nor_9 (nor_9_out, d_ff_18_q, not_18_out);
  nor nor_10 (nor_10_out, d_ff_19_q, not_19_out);
  nor nor_11 (nor_11_out, d_ff_20_q, not_20_out);
  nor nor_12 (nor_12_out, d_ff_21_q, not_21_out);
  nor nor_13 (nor_13_out, d_ff_22_q, not_22_out);
  not not_23 (not_23_out, FOUT);
  D_Flip_Flop d_ff_34 (.clk(nACLK), .D(nor_13_out), .Qn(FOUT));  // open: Q, preset, en, reset

  // Notes on the sheet:
  //   FSTEP
  //   FLOAD
  //   NOR1
  //   NOR2
  //   INV1
  //   DL1
endmodule
// TRIANGLE LINEAR COUNTER
module TRIANGLE_LINEAR_COUNTER (
  input  nACLK,
  input  ACLK,
  input  W4008,
  input  W400B,
  input  nLFO1,
  input  RES,
  input  D0,
  input  D1,
  input  D2,
  input  D3,
  input  D4,
  input  D5,
  input  D6,
  input  D7,
  output OUT,
  output TRI_LC
);

  wire and_1_out, and_2_out, and_3_out, and_4_out, and_5_out, and_6_out, and_7_out, and_8_out, and_9_out,
       and_10_out, and_11_out, and_12_out, and_13_out, and_14_out, and_15_out, d_ff_1_q, d_ff_2_q, d_ff_3_q,
       d_ff_4_q, d_ff_5_q, d_ff_6_q, d_ff_7_q, d_ff_8_q, d_ff_9_q, d_ff_10_q, d_ff_11_qn, d_ff_12_q,
       d_ff_12_qn, d_ff_13_q, d_ff_13_qn, d_ff_14_q, d_ff_14_qn, d_ff_15_q, d_ff_15_qn, d_ff_16_q,
       d_ff_16_qn, d_ff_17_q, d_ff_17_qn, d_ff_18_q, d_ff_18_qn, d_ff_19_qn, d_ff_20_qn, d_ff_21_qn,
       d_ff_22_qn, d_ff_23_qn, d_ff_24_qn, d_ff_25_qn, d_ff_26_q, multiplexer_1_out, multiplexer_2_out,
       multiplexer_3_out, multiplexer_4_out, multiplexer_5_out, multiplexer_6_out, multiplexer_7_out,
       nor_1_out, nor_2_out, nor_3_out, nor_4_out, nor_5_out, nor_6_out, nor_7_out, nor_8_out, nor_9_out,
       nor_10_out, nor_12_out, not_1_out, not_2_out, not_3_out, not_4_out, not_5_out, not_6_out, not_7_out,
       not_8_out, not_9_out, not_10_out, not_11_out, not_12_out, not_13_out, not_14_out, or_1_out, or_2_out,
       or_3_out, or_4_out, or_5_out, or_6_out, or_7_out;

  and and_1 (and_1_out, ACLK, W4008);
  D_Flip_Flop #(.trigger("high")) d_ff_1 (.clk(and_1_out), .D(D0), .Q(d_ff_1_q));  // open: Qn, preset, en, reset
  D_Flip_Flop #(.trigger("high")) d_ff_2 (.clk(and_1_out), .D(D1), .Q(d_ff_2_q));  // open: Qn, preset, en, reset
  D_Flip_Flop #(.trigger("high")) d_ff_3 (.clk(and_1_out), .D(D2), .Q(d_ff_3_q));  // open: Qn, preset, en, reset
  D_Flip_Flop #(.trigger("high")) d_ff_4 (.clk(and_1_out), .D(D3), .Q(d_ff_4_q));  // open: Qn, preset, en, reset
  D_Flip_Flop #(.trigger("high")) d_ff_5 (.clk(and_1_out), .D(D4), .Q(d_ff_5_q));  // open: Qn, preset, en, reset
  D_Flip_Flop #(.trigger("high")) d_ff_6 (.clk(and_1_out), .D(D5), .Q(d_ff_6_q));  // open: Qn, preset, en, reset
  D_Flip_Flop #(.trigger("high")) d_ff_7 (.clk(and_1_out), .D(D6), .Q(d_ff_7_q));  // open: Qn, preset, en, reset
  D_Flip_Flop #(.trigger("high")) d_ff_8 (
    .clk(and_1_out), .D(D7), .Q(d_ff_8_q), .Qn(TRI_LC));  // open: preset, en, reset
  not not_1 (not_1_out, d_ff_1_q);
  not not_2 (not_2_out, d_ff_2_q);
  not not_3 (not_3_out, d_ff_3_q);
  not not_4 (not_4_out, d_ff_4_q);
  not not_5 (not_5_out, d_ff_5_q);
  not not_6 (not_6_out, d_ff_6_q);
  not not_7 (not_7_out, d_ff_7_q);
  and and_2 (and_2_out, nor_4_out, d_ff_1_q);
  and and_3 (and_3_out, nor_4_out, not_1_out);
  and and_4 (and_4_out, nor_4_out, d_ff_2_q);
  and and_5 (and_5_out, nor_4_out, not_2_out);
  and and_6 (and_6_out, nor_4_out, d_ff_3_q);
  and and_7 (and_7_out, nor_4_out, not_3_out);
  and and_8 (and_8_out, nor_4_out, d_ff_4_q);
  and and_9 (and_9_out, nor_4_out, not_4_out);
  and and_10 (and_10_out, nor_4_out, d_ff_5_q);
  and and_11 (and_11_out, nor_4_out, not_5_out);
  and and_12 (and_12_out, nor_4_out, d_ff_6_q);
  and and_13 (and_13_out, nor_4_out, not_6_out);
  and and_14 (and_14_out, nor_4_out, d_ff_7_q);
  and and_15 (and_15_out, nor_4_out, not_7_out);
  D_Flip_Flop d_ff_9 (.clk(nACLK), .D(OUT), .Q(d_ff_9_q));  // open: Qn, preset, en, reset
  D_Flip_Flop d_ff_10 (.clk(nACLK), .D(nor_2_out), .Q(d_ff_10_q));  // open: Qn, preset, en, reset
  D_Flip_Flop d_ff_11 (.clk(nACLK), .D(nor_2_out), .Qn(d_ff_11_qn));  // open: Q, preset, en, reset
  D_Flip_Flop d_ff_12 (
    .clk(nor_3_out), .D(d_ff_19_qn), .Q(d_ff_12_q), .Qn(d_ff_12_qn), .preset(and_2_out), .reset(or_1_out));  // open: en
  or or_1 (or_1_out, and_3_out, RES);
  D_Flip_Flop d_ff_13 (
    .clk(nor_3_out), .D(d_ff_20_qn), .Q(d_ff_13_q), .Qn(d_ff_13_qn), .preset(and_4_out), .reset(or_2_out));  // open: en
  or or_2 (or_2_out, and_5_out, RES);
  D_Flip_Flop d_ff_14 (
    .clk(nor_3_out), .D(d_ff_21_qn), .Q(d_ff_14_q), .Qn(d_ff_14_qn), .preset(and_6_out), .reset(or_3_out));  // open: en
  or or_3 (or_3_out, and_7_out, RES);
  D_Flip_Flop d_ff_15 (
    .clk(nor_3_out), .D(d_ff_22_qn), .Q(d_ff_15_q), .Qn(d_ff_15_qn), .preset(and_8_out), .reset(or_4_out));  // open: en
  or or_4 (or_4_out, and_9_out, RES);
  D_Flip_Flop d_ff_16 (
    .clk(nor_3_out), .D(d_ff_23_qn), .Q(d_ff_16_q), .Qn(d_ff_16_qn), .preset(and_10_out), .reset(or_5_out));  // open: en
  or or_5 (or_5_out, and_11_out, RES);
  D_Flip_Flop d_ff_17 (
    .clk(nor_3_out), .D(d_ff_24_qn), .Q(d_ff_17_q), .Qn(d_ff_17_qn), .preset(and_12_out), .reset(or_6_out));  // open: en
  or or_6 (or_6_out, and_13_out, RES);
  D_Flip_Flop d_ff_18 (
    .clk(nor_3_out), .D(d_ff_25_qn), .Q(d_ff_18_q), .Qn(d_ff_18_qn), .preset(and_14_out), .reset(or_7_out));  // open: en
  or or_7 (or_7_out, and_15_out, RES);
  nor nor_1 (nor_1_out, W400B, nor_2_out);
  nor nor_2 (nor_2_out, nor_1_out, nor_12_out);
  nor nor_3 (nor_3_out, d_ff_9_q, nLFO1, d_ff_10_q);
  nor nor_4 (nor_4_out, nLFO1, d_ff_11_qn);
  Multiplexer multiplexer_1 (.in0(d_ff_12_qn), .in1(d_ff_12_q), .out(multiplexer_1_out), .sel(1'b1));  // open: en
  Multiplexer multiplexer_2 (.in0(d_ff_13_qn), .in1(d_ff_13_q), .out(multiplexer_2_out), .sel(nor_5_out));  // open: en
  Multiplexer multiplexer_3 (.in0(d_ff_14_qn), .in1(d_ff_14_q), .out(multiplexer_3_out), .sel(nor_6_out));  // open: en
  Multiplexer multiplexer_4 (.in0(d_ff_15_qn), .in1(d_ff_15_q), .out(multiplexer_4_out), .sel(nor_7_out));  // open: en
  Multiplexer multiplexer_5 (.in0(d_ff_16_qn), .in1(d_ff_16_q), .out(multiplexer_5_out), .sel(nor_8_out));  // open: en
  Multiplexer multiplexer_6 (.in0(d_ff_17_qn), .in1(d_ff_17_q), .out(multiplexer_6_out), .sel(nor_9_out));  // open: en
  Multiplexer multiplexer_7 (.in0(d_ff_18_qn), .in1(d_ff_18_q), .out(multiplexer_7_out), .sel(nor_10_out));  // open: en
  D_Flip_Flop d_ff_19 (.clk(nACLK), .D(multiplexer_1_out), .Qn(d_ff_19_qn));  // open: Q, preset, en, reset
  not not_8 (not_8_out, 1'b1);
  D_Flip_Flop d_ff_20 (.clk(nACLK), .D(multiplexer_2_out), .Qn(d_ff_20_qn));  // open: Q, preset, en, reset
  not not_9 (not_9_out, nor_5_out);
  D_Flip_Flop d_ff_21 (.clk(nACLK), .D(multiplexer_3_out), .Qn(d_ff_21_qn));  // open: Q, preset, en, reset
  not not_10 (not_10_out, nor_6_out);
  D_Flip_Flop d_ff_22 (.clk(nACLK), .D(multiplexer_4_out), .Qn(d_ff_22_qn));  // open: Q, preset, en, reset
  not not_11 (not_11_out, nor_7_out);
  D_Flip_Flop d_ff_23 (.clk(nACLK), .D(multiplexer_5_out), .Qn(d_ff_23_qn));  // open: Q, preset, en, reset
  not not_12 (not_12_out, nor_8_out);
  D_Flip_Flop d_ff_24 (.clk(nACLK), .D(multiplexer_6_out), .Qn(d_ff_24_qn));  // open: Q, preset, en, reset
  not not_13 (not_13_out, nor_9_out);
  D_Flip_Flop d_ff_25 (.clk(nACLK), .D(multiplexer_7_out), .Qn(d_ff_25_qn));  // open: Q, preset, en, reset
  not not_14 (not_14_out, nor_10_out);
  D_Flip_Flop d_ff_26 (.clk(nACLK), .D(nor_1_out), .Q(d_ff_26_q));  // open: Qn, preset, en, reset
  nor nor_5 (nor_5_out, d_ff_12_q, not_8_out);
  nor nor_6 (nor_6_out, d_ff_13_q, not_9_out);
  nor nor_7 (nor_7_out, d_ff_14_q, not_10_out);
  nor nor_8 (nor_8_out, d_ff_15_q, not_11_out);
  nor nor_9 (nor_9_out, d_ff_16_q, not_12_out);
  nor nor_10 (nor_10_out, d_ff_17_q, not_13_out);
  nor nor_11 (OUT, d_ff_18_q, not_14_out);
  nor nor_12 (nor_12_out, d_ff_26_q, nLFO1, d_ff_8_q);

  // Notes on the sheet:
  //   DL4
  //   DL3
  //   DL2
  //   NORFF1
  //   RS1
  //   NORFF2
  //   NOR5
  //   STEP
  //   NOR4
  //   LOAD
  //   DL5
  //   NOR6
endmodule

module TRIANGLE_OUTPUT_COUNTER (
  input  PHI1,
  input  RES,
  input  TSTEP,
  output TRI0,
  output TRI1,
  output TRI2,
  output TRI3
);

  wire d_ff_1_q, d_ff_1_qn, d_ff_2_q, d_ff_2_qn, d_ff_3_q, d_ff_3_qn, d_ff_4_q, d_ff_4_qn, d_ff_5_q,
       d_ff_5_qn, d_ff_6_qn, d_ff_7_qn, d_ff_8_qn, d_ff_9_qn, d_ff_10_qn, multiplexer_1_out,
       multiplexer_2_out, multiplexer_3_out, multiplexer_4_out, multiplexer_5_out, multiplexer_6_out,
       multiplexer_7_out, multiplexer_8_out, multiplexer_9_out, nor_1_out, nor_2_out, nor_3_out, nor_4_out,
       not_1_out, not_2_out, not_3_out, not_4_out;

  D_Flip_Flop d_ff_1 (.clk(TSTEP), .D(d_ff_6_qn), .Q(d_ff_1_q), .Qn(d_ff_1_qn), .reset(RES));  // open: preset, en
  D_Flip_Flop d_ff_2 (.clk(TSTEP), .D(d_ff_7_qn), .Q(d_ff_2_q), .Qn(d_ff_2_qn), .reset(RES));  // open: preset, en
  D_Flip_Flop d_ff_3 (.clk(TSTEP), .D(d_ff_8_qn), .Q(d_ff_3_q), .Qn(d_ff_3_qn), .reset(RES));  // open: preset, en
  D_Flip_Flop d_ff_4 (.clk(TSTEP), .D(d_ff_9_qn), .Q(d_ff_4_q), .Qn(d_ff_4_qn), .reset(RES));  // open: preset, en
  D_Flip_Flop d_ff_5 (.clk(TSTEP), .D(d_ff_10_qn), .Q(d_ff_5_q), .Qn(d_ff_5_qn), .reset(RES));  // open: preset, en
  Multiplexer #(.enable("false")) multiplexer_1 (.in0(d_ff_1_qn), .in1(d_ff_1_q), .out(multiplexer_1_out), .sel(1'b1));
  Multiplexer #(.enable("false")) multiplexer_2 (
    .in0(d_ff_2_qn), .in1(d_ff_2_q), .out(multiplexer_2_out), .sel(nor_1_out));
  Multiplexer #(.enable("false")) multiplexer_3 (
    .in0(d_ff_3_qn), .in1(d_ff_3_q), .out(multiplexer_3_out), .sel(nor_2_out));
  Multiplexer #(.enable("false")) multiplexer_4 (
    .in0(d_ff_4_qn), .in1(d_ff_4_q), .out(multiplexer_4_out), .sel(nor_3_out));
  Multiplexer #(.enable("false")) multiplexer_5 (
    .in0(d_ff_5_qn), .in1(d_ff_5_q), .out(multiplexer_5_out), .sel(nor_4_out));
  D_Flip_Flop d_ff_6 (.clk(PHI1), .D(multiplexer_1_out), .Qn(d_ff_6_qn));  // open: Q, preset, en, reset
  not not_1 (not_1_out, 1'b1);
  D_Flip_Flop d_ff_7 (.clk(PHI1), .D(multiplexer_2_out), .Qn(d_ff_7_qn));  // open: Q, preset, en, reset
  not not_2 (not_2_out, nor_1_out);
  D_Flip_Flop d_ff_8 (.clk(PHI1), .D(multiplexer_3_out), .Qn(d_ff_8_qn));  // open: Q, preset, en, reset
  not not_3 (not_3_out, nor_2_out);
  D_Flip_Flop d_ff_9 (.clk(PHI1), .D(multiplexer_4_out), .Qn(d_ff_9_qn));  // open: Q, preset, en, reset
  not not_4 (not_4_out, nor_3_out);
  D_Flip_Flop d_ff_10 (.clk(PHI1), .D(multiplexer_5_out), .Qn(d_ff_10_qn));  // open: Q, preset, en, reset
  nor nor_1 (nor_1_out, d_ff_1_qn, not_1_out);
  nor nor_2 (nor_2_out, d_ff_2_qn, not_2_out);
  nor nor_3 (nor_3_out, d_ff_3_qn, not_3_out);
  nor nor_4 (nor_4_out, d_ff_4_qn, not_4_out);
  Multiplexer #(.enable("false")) multiplexer_6 (
    .in0(d_ff_1_q), .in1(d_ff_1_qn), .out(multiplexer_6_out), .sel(d_ff_5_q));
  not not_5 (TRI0, multiplexer_6_out);
  not not_6 (TRI1, multiplexer_7_out);
  Multiplexer #(.enable("false")) multiplexer_7 (
    .in0(d_ff_2_q), .in1(d_ff_2_qn), .out(multiplexer_7_out), .sel(d_ff_5_q));
  Multiplexer #(.enable("false")) multiplexer_8 (
    .in0(d_ff_3_q), .in1(d_ff_3_qn), .out(multiplexer_8_out), .sel(d_ff_5_q));
  not not_7 (TRI2, multiplexer_8_out);
  Multiplexer #(.enable("false")) multiplexer_9 (
    .in0(d_ff_4_q), .in1(d_ff_4_qn), .out(multiplexer_9_out), .sel(d_ff_5_q));
  not not_8 (TRI3, multiplexer_9_out);
endmodule

// NOISE CHANNEL
module NOISE_CHANNEL (
  input  ACLK,
  input  nACLK,
  input  D7,
  input  D6,
  input  D5,
  input  D4,
  input  D3,
  input  D2,
  input  D1,
  input  D0,
  input  W400E,
  input  W400F,
  input  Res,
  input  NORND,
  input  nLFO1,
  input  W400C,
  output RND0,
  output RND1,
  output RND2,
  output RND3
);

  wire and_1_out, and_2_out, d_latch_1_q, d_latch_2_q, d_latch_3_q, d_latch_4_q, d_latch_5_q, d_latch_6_q,
       d_latch_7_q, d_latch_8_q, d_latch_9_q, d_latch_10_not_q, frequency_lfsr_1_fload, multiplexer_1_out,
       multiplexer_2_out, multiplexer_3_out, multiplexer_4_out, noise_envelope_control_1_eres,
       noise_envelope_control_1_estep, noise_envelope_control_1_load, noise_envelope_control_1_output_oec,
       noise_envelope_control_1_reload, noise_envelope_control_1_step,
       noise_envelope_frequency_divider_1_output, noise_envelope_output_counter_1_env0,
       noise_envelope_output_counter_1_env1, noise_envelope_output_counter_1_env2,
       noise_envelope_output_counter_1_env3, noise_envelope_output_counter_1_output_oec, noise_lfsr_1_rndout,
       not_1_out, not_2_out, not_3_out, not_4_out, not_5_out;

  and and_1 (and_1_out, ACLK, W400E);
  D_latch d_latch_1 (.EN(and_1_out), .D(D3), .Q(d_latch_1_q));  // open: NOT_Q
  D_latch d_latch_2 (.EN(and_1_out), .D(D2), .Q(d_latch_2_q));  // open: NOT_Q
  D_latch d_latch_3 (.EN(and_1_out), .D(D1), .Q(d_latch_3_q));  // open: NOT_Q
  D_latch d_latch_4 (.EN(and_1_out), .D(D0), .Q(d_latch_4_q));  // open: NOT_Q
  and and_2 (and_2_out, ACLK, W400C);
  D_latch d_latch_5 (.EN(and_2_out), .D(D0), .Q(d_latch_5_q));  // open: NOT_Q
  D_latch d_latch_6 (.EN(and_2_out), .D(D1), .Q(d_latch_6_q));  // open: NOT_Q
  D_latch d_latch_7 (.EN(and_2_out), .D(D2), .Q(d_latch_7_q));  // open: NOT_Q
  D_latch d_latch_8 (.EN(and_2_out), .D(D3), .Q(d_latch_8_q));  // open: NOT_Q
  D_latch d_latch_9 (.EN(and_2_out), .D(D4), .Q(d_latch_9_q));  // open: NOT_Q
  D_latch d_latch_10 (.EN(and_2_out), .D(D5), .NOT_Q(d_latch_10_not_q));  // open: Q
  not not_1 (not_1_out, ACLK);
  FREQUENCY_LFSR frequency_lfsr_1 (
    .nACLK(nACLK), .nACLK1(not_1_out), .RES(Res), .F0(d_latch_4_q), .F1(d_latch_3_q), .F2(d_latch_2_q),
    .F3(d_latch_1_q), .FLOAD(frequency_lfsr_1_fload));
  NOISE_LFSR noise_lfsr_1 (
    .RSTEP(frequency_lfsr_1_fload), .ACLK(ACLK), .W400E(W400E), .D7(D7), .NORND(NORND),
    .RNDOUT(noise_lfsr_1_rndout));
  NOISE_ENVELOPE_FREQUENCY_DIVIDER noise_envelope_frequency_divider_1 (
    .nACLK(nACLK), .LOAD(d_latch_5_q), .STEP(noise_envelope_control_1_load),
    .RES(noise_envelope_control_1_step), .Vol0(Res), .Vol1(d_latch_6_q), .Vol2(d_latch_7_q),
    .Vol3(d_latch_8_q), .Output(noise_envelope_frequency_divider_1_output));
  NOISE_ENVELOPE_CONTROL noise_envelope_control_1 (
    .nACLK(nACLK), .nLFO1(nLFO1), .W400F(W400F), .Input_ERC(noise_envelope_frequency_divider_1_output),
    .Input_OEC(noise_envelope_output_counter_1_output_oec), .RND_LC(d_latch_10_not_q),
    .RELOAD(noise_envelope_control_1_reload), .LOAD(noise_envelope_control_1_load),
    .STEP(noise_envelope_control_1_step), .Estep(noise_envelope_control_1_estep),
    .Eres(noise_envelope_control_1_eres), .Output_OEC(noise_envelope_control_1_output_oec));
  NOISE_ENVELOPE_OUTPUT_COUNTER noise_envelope_output_counter_1 (
    .nACLK(nACLK), .Input_OEC(noise_envelope_control_1_output_oec), .Eres(noise_envelope_control_1_eres),
    .Estep(noise_envelope_control_1_estep), .RES(Res), .Reload(noise_envelope_control_1_reload),
    .Env0(noise_envelope_output_counter_1_env0), .Env1(noise_envelope_output_counter_1_env1),
    .Env2(noise_envelope_output_counter_1_env2), .Env3(noise_envelope_output_counter_1_env3),
    .Output_OEC(noise_envelope_output_counter_1_output_oec));
  not not_2 (not_2_out, multiplexer_1_out);
  Multiplexer #(.enable("false")) multiplexer_1 (
    .in0(noise_envelope_output_counter_1_env0), .in1(d_latch_5_q), .out(multiplexer_1_out), .sel(d_latch_9_q));
  Multiplexer #(.enable("false")) multiplexer_2 (
    .in0(noise_envelope_output_counter_1_env1), .in1(d_latch_6_q), .out(multiplexer_2_out), .sel(d_latch_9_q));
  not not_3 (not_3_out, multiplexer_2_out);
  Multiplexer #(.enable("false")) multiplexer_3 (
    .in0(noise_envelope_output_counter_1_env2), .in1(d_latch_7_q), .out(multiplexer_3_out), .sel(d_latch_9_q));
  not not_4 (not_4_out, multiplexer_3_out);
  Multiplexer #(.enable("false")) multiplexer_4 (
    .in0(noise_envelope_output_counter_1_env3), .in1(d_latch_8_q), .out(multiplexer_4_out), .sel(d_latch_9_q));
  not not_5 (not_5_out, multiplexer_4_out);
  nor nor_1 (RND0, not_2_out, noise_lfsr_1_rndout);
  nor nor_2 (RND1, not_3_out, noise_lfsr_1_rndout);
  nor nor_3 (RND2, not_4_out, noise_lfsr_1_rndout);
  nor nor_4 (RND3, not_5_out, noise_lfsr_1_rndout);

  // Notes on the sheet:
  //   F3
  //   F2
  //   F1
  //   F0
  //   Vol0
  //   Vol1
  //   Vol2
  //   Vol3
endmodule

// FREQUENCY LFSR
module FREQUENCY_LFSR (
  input  nACLK,
  input  nACLK1,
  input  RES,
  input  F0,
  input  F1,
  input  F2,
  input  F3,
  output FLOAD
);

  wire and_1_out, and_2_out, and_3_out, and_4_out, and_5_out, and_6_out, and_7_out, and_8_out, and_9_out,
       and_10_out, and_11_out, and_12_out, and_13_out, and_14_out, and_15_out, and_16_out, and_17_out,
       and_18_out, and_19_out, and_20_out, and_21_out, and_22_out, and_23_out, d_ff_1_qn, d_ff_2_qn,
       d_ff_3_qn, d_ff_4_qn, d_ff_5_qn, d_ff_6_qn, d_ff_7_qn, d_ff_8_qn, d_ff_9_qn, d_ff_10_qn, d_ff_11_qn,
       d_ff_12_qn, d_ff_13_qn, d_ff_14_qn, d_ff_15_qn, d_ff_16_qn, d_ff_17_qn, d_ff_18_qn, d_ff_19_qn,
       d_ff_20_qn, d_ff_21_qn, d_ff_22_qn, noise_table_1_lp0, noise_table_1_lp1, noise_table_1_lp2,
       noise_table_1_lp3, noise_table_1_lp4, noise_table_1_lp5, noise_table_1_lp6, noise_table_1_lp7,
       noise_table_1_lp8, noise_table_1_lp9, noise_table_1_lp10, nor_1_out, nor_3_out, nor_4_out, nor_5_out,
       nor_6_out, nor_7_out, not_1_out, not_2_out, not_3_out, not_4_out, not_5_out, not_6_out, not_7_out,
       not_8_out, not_9_out, not_10_out, not_11_out, not_12_out, not_13_out, not_14_out, not_15_out;

  NOISE_TABLE noise_table_1 (
    .LP0(noise_table_1_lp0), .LP1(noise_table_1_lp1), .LP2(noise_table_1_lp2), .LP3(noise_table_1_lp3),
    .LP4(noise_table_1_lp4), .LP5(noise_table_1_lp5), .LP6(noise_table_1_lp6), .LP7(noise_table_1_lp7),
    .LP8(noise_table_1_lp8), .LP9(noise_table_1_lp9), .LP10(noise_table_1_lp10), .F3(F3), .F2(F2), .F1(F1),
    .F0(F0));
  not not_1 (not_1_out, nACLK1);
  nor nor_1 (nor_1_out, not_1_out, nor_5_out);
  not not_2 (not_2_out, nor_5_out);
  nor nor_2 (FLOAD, not_2_out, not_1_out);
  nor nor_3 (nor_3_out, nor_6_out, d_ff_22_qn, d_ff_20_qn);
  and and_1 (and_1_out, d_ff_22_qn, d_ff_20_qn);
  not not_3 (not_3_out, noise_table_1_lp0);
  not not_4 (not_4_out, noise_table_1_lp1);
  not not_5 (not_5_out, noise_table_1_lp2);
  not not_6 (not_6_out, noise_table_1_lp3);
  not not_7 (not_7_out, noise_table_1_lp4);
  not not_8 (not_8_out, noise_table_1_lp5);
  not not_9 (not_9_out, noise_table_1_lp6);
  not not_10 (not_10_out, noise_table_1_lp7);
  not not_11 (not_11_out, noise_table_1_lp8);
  not not_12 (not_12_out, noise_table_1_lp9);
  not not_13 (not_13_out, noise_table_1_lp10);
  nor nor_4 (nor_4_out, nor_3_out, RES, and_1_out);
  and and_2 (and_2_out, FLOAD, noise_table_1_lp0);
  and and_3 (and_3_out, FLOAD, not_3_out);
  and and_4 (and_4_out, FLOAD, noise_table_1_lp1);
  and and_5 (and_5_out, FLOAD, not_4_out);
  and and_6 (and_6_out, FLOAD, noise_table_1_lp2);
  and and_7 (and_7_out, FLOAD, not_5_out);
  and and_8 (and_8_out, FLOAD, noise_table_1_lp3);
  and and_9 (and_9_out, FLOAD, not_6_out);
  and and_10 (and_10_out, FLOAD, noise_table_1_lp4);
  and and_11 (and_11_out, FLOAD, not_7_out);
  and and_12 (and_12_out, FLOAD, noise_table_1_lp5);
  and and_13 (and_13_out, FLOAD, not_8_out);
  and and_14 (and_14_out, FLOAD, noise_table_1_lp6);
  and and_15 (and_15_out, FLOAD, not_9_out);
  and and_16 (and_16_out, FLOAD, noise_table_1_lp7);
  and and_17 (and_17_out, FLOAD, not_10_out);
  and and_18 (and_18_out, FLOAD, noise_table_1_lp8);
  and and_19 (and_19_out, FLOAD, not_11_out);
  and and_20 (and_20_out, FLOAD, noise_table_1_lp9);
  and and_21 (and_21_out, FLOAD, not_12_out);
  and and_22 (and_22_out, FLOAD, noise_table_1_lp10);
  and and_23 (and_23_out, FLOAD, not_13_out);
  D_Flip_Flop d_ff_1 (
    .clk(nor_1_out), .D(nor_4_out), .Qn(d_ff_1_qn), .preset(and_2_out), .reset(and_3_out));  // open: Q, en
  D_Flip_Flop d_ff_2 (
    .clk(nor_1_out), .D(d_ff_12_qn), .Qn(d_ff_2_qn), .preset(and_4_out), .reset(and_5_out));  // open: Q, en
  D_Flip_Flop d_ff_3 (
    .clk(nor_1_out), .D(d_ff_13_qn), .Qn(d_ff_3_qn), .preset(and_6_out), .reset(and_7_out));  // open: Q, en
  D_Flip_Flop d_ff_4 (
    .clk(nor_1_out), .D(d_ff_14_qn), .Qn(d_ff_4_qn), .preset(and_8_out), .reset(and_9_out));  // open: Q, en
  D_Flip_Flop d_ff_5 (
    .clk(nor_1_out), .D(d_ff_15_qn), .Qn(d_ff_5_qn), .preset(and_10_out), .reset(and_11_out));  // open: Q, en
  D_Flip_Flop d_ff_6 (
    .clk(nor_1_out), .D(d_ff_16_qn), .Qn(d_ff_6_qn), .preset(and_12_out), .reset(and_13_out));  // open: Q, en
  D_Flip_Flop d_ff_7 (
    .clk(nor_1_out), .D(d_ff_17_qn), .Qn(d_ff_7_qn), .preset(and_14_out), .reset(and_15_out));  // open: Q, en
  D_Flip_Flop d_ff_8 (
    .clk(nor_1_out), .D(d_ff_18_qn), .Qn(d_ff_8_qn), .preset(and_16_out), .reset(and_17_out));  // open: Q, en
  D_Flip_Flop d_ff_9 (
    .clk(nor_1_out), .D(d_ff_19_qn), .Qn(d_ff_9_qn), .preset(and_18_out), .reset(and_19_out));  // open: Q, en
  D_Flip_Flop d_ff_10 (
    .clk(nor_1_out), .D(d_ff_20_qn), .Qn(d_ff_10_qn), .preset(and_20_out), .reset(and_21_out));  // open: Q, en
  D_Flip_Flop d_ff_11 (
    .clk(nor_1_out), .D(d_ff_21_qn), .Qn(d_ff_11_qn), .preset(and_22_out), .reset(and_23_out));  // open: Q, en
  D_Flip_Flop d_ff_12 (.clk(nACLK), .D(d_ff_1_qn), .Qn(d_ff_12_qn));  // open: Q, preset, en, reset
  D_Flip_Flop d_ff_13 (.clk(nACLK), .D(d_ff_2_qn), .Qn(d_ff_13_qn));  // open: Q, preset, en, reset
  D_Flip_Flop d_ff_14 (.clk(nACLK), .D(d_ff_3_qn), .Qn(d_ff_14_qn));  // open: Q, preset, en, reset
  D_Flip_Flop d_ff_15 (.clk(nACLK), .D(d_ff_4_qn), .Qn(d_ff_15_qn));  // open: Q, preset, en, reset
  D_Flip_Flop d_ff_16 (.clk(nACLK), .D(d_ff_5_qn), .Qn(d_ff_16_qn));  // open: Q, preset, en, reset
  D_Flip_Flop d_ff_17 (.clk(nACLK), .D(d_ff_6_qn), .Qn(d_ff_17_qn));  // open: Q, preset, en, reset
  D_Flip_Flop d_ff_18 (.clk(nACLK), .D(d_ff_7_qn), .Qn(d_ff_18_qn));  // open: Q, preset, en, reset
  D_Flip_Flop d_ff_19 (.clk(nACLK), .D(d_ff_8_qn), .Qn(d_ff_19_qn));  // open: Q, preset, en, reset
  D_Flip_Flop d_ff_20 (.clk(nACLK), .D(d_ff_9_qn), .Qn(d_ff_20_qn));  // open: Q, preset, en, reset
  D_Flip_Flop d_ff_21 (.clk(nACLK), .D(d_ff_10_qn), .Qn(d_ff_21_qn));  // open: Q, preset, en, reset
  D_Flip_Flop d_ff_22 (.clk(nACLK), .D(d_ff_11_qn), .Qn(d_ff_22_qn));  // open: Q, preset, en, reset
  not not_14 (not_14_out, d_ff_22_qn);
  nor nor_5 (nor_5_out, not_15_out, RES);
  nor nor_6 (nor_6_out, d_ff_12_qn, d_ff_13_qn, d_ff_14_qn, d_ff_15_qn, d_ff_16_qn, d_ff_17_qn, d_ff_18_qn, d_ff_19_qn, d_ff_20_qn, d_ff_21_qn, d_ff_22_qn);
  nor nor_7 (nor_7_out, d_ff_12_qn, d_ff_13_qn, d_ff_14_qn, d_ff_15_qn, d_ff_16_qn, d_ff_17_qn, d_ff_18_qn, d_ff_19_qn, d_ff_20_qn, d_ff_21_qn, not_14_out);
  not not_15 (not_15_out, nor_7_out);

  // Notes on the sheet:
  //   NOR1
  //   NOR2
  //   INV3
  //   NOR3
endmodule

// NOISE TABLE
module NOISE_TABLE (
  input  F3,
  input  F2,
  input  F1,
  input  F0,
  output LP0,
  output LP1,
  output LP2,
  output LP3,
  output LP4,
  output LP5,
  output LP6,
  output LP7,
  output LP8,
  output LP9,
  output LP10
);

  wire not_1_out, not_2_out, not_3_out, not_4_out, transistor_19_out, transistor_20_out, transistor_33_out,
       transistor_52_out, transistor_62_out, transistor_63_out, transistor_78_out, transistor_88_out,
       transistor_105_out, transistor_114_out, transistor_115_out, transistor_128_out, transistor_143_out,
       transistor_156_out, transistor_157_out, transistor_174_out;

  Transistor #(.\type ("n"), .gate("br")) transistor_1 (.in(1'b0), .out(LP0), .gate(transistor_20_out));
  Transistor #(.\type ("n"), .gate("br")) transistor_2 (.in(1'b0), .out(LP1), .gate(transistor_20_out));
  Transistor #(.\type ("n"), .gate("br")) transistor_3 (.in(1'b0), .out(LP3), .gate(transistor_20_out));
  Transistor #(.\type ("n"), .gate("br")) transistor_4 (.in(1'b0), .out(LP5), .gate(transistor_20_out));
  Transistor #(.\type ("n"), .gate("br")) transistor_5 (.in(1'b0), .out(LP6), .gate(transistor_20_out));
  Transistor #(.\type ("n"), .gate("br")) transistor_6 (.in(1'b0), .out(LP7), .gate(transistor_20_out));
  Transistor #(.\type ("n"), .gate("br")) transistor_7 (.in(1'b0), .out(LP8), .gate(transistor_20_out));
  Transistor #(.\type ("n"), .gate("br")) transistor_8 (.in(1'b0), .out(LP9), .gate(transistor_20_out));
  Transistor #(.\type ("n"), .gate("br")) transistor_9 (.in(1'b0), .out(LP10), .gate(transistor_20_out));
  not not_1 (not_1_out, F3);
  not not_2 (not_2_out, F2);
  not not_3 (not_3_out, F1);
  not not_4 (not_4_out, F0);
  Transistor #(.\type ("n"), .gate("br")) transistor_10 (.in(1'b0), .out(LP0), .gate(transistor_19_out));
  Transistor #(.\type ("n"), .gate("br")) transistor_11 (.in(1'b0), .out(LP3), .gate(transistor_19_out));
  Transistor #(.\type ("n"), .gate("br")) transistor_12 (.in(1'b0), .out(LP4), .gate(transistor_19_out));
  Transistor #(.\type ("n"), .gate("br")) transistor_13 (.in(1'b0), .out(LP5), .gate(transistor_19_out));
  Transistor #(.\type ("n"), .gate("br")) transistor_14 (.in(1'b0), .out(LP6), .gate(transistor_19_out));
  Transistor #(.\type ("n"), .gate("br")) transistor_15 (.in(1'b0), .out(LP7), .gate(transistor_19_out));
  Transistor #(.\type ("n"), .gate("br")) transistor_16 (.in(1'b0), .out(LP8), .gate(transistor_19_out));
  Transistor #(.\type ("n"), .gate("br")) transistor_17 (.in(1'b0), .out(LP9), .gate(transistor_19_out));
  Transistor #(.\type ("n"), .gate("br")) transistor_18 (.in(1'b0), .out(LP10), .gate(transistor_19_out));
  Transistor #(.\type ("n")) transistor_19 (.in(1'b0), .out(transistor_19_out), .gate(not_1_out));
  Transistor #(.\type ("n")) transistor_20 (.in(1'b0), .out(transistor_20_out), .gate(not_1_out));
  Transistor #(.\type ("n")) transistor_21 (.in(1'b0), .out(transistor_19_out), .gate(not_2_out));
  Transistor #(.\type ("n")) transistor_22 (.in(1'b0), .out(transistor_20_out), .gate(not_2_out));
  Transistor #(.\type ("n")) transistor_23 (.in(1'b0), .out(transistor_19_out), .gate(not_3_out));
  Transistor #(.\type ("n")) transistor_24 (.in(1'b0), .out(transistor_20_out), .gate(not_3_out));
  Transistor #(.\type ("n")) transistor_25 (.in(1'b0), .out(transistor_19_out), .gate(F0));
  Transistor #(.\type ("n")) transistor_26 (.in(1'b0), .out(transistor_20_out), .gate(not_4_out));
  Pull_Resistor #(.pull(1)) pull_resistor_1 (.node(transistor_19_out));
  Pull_Resistor #(.pull(1)) pull_resistor_2 (.node(transistor_20_out));
  Transistor #(.\type ("n"), .gate("br")) transistor_27 (.in(1'b0), .out(LP0), .gate(transistor_33_out));
  Transistor #(.\type ("n"), .gate("br")) transistor_28 (.in(1'b0), .out(LP2), .gate(transistor_33_out));
  Transistor #(.\type ("n"), .gate("br")) transistor_29 (.in(1'b0), .out(LP3), .gate(transistor_33_out));
  Transistor #(.\type ("n"), .gate("br")) transistor_30 (.in(1'b0), .out(LP4), .gate(transistor_33_out));
  Transistor #(.\type ("n"), .gate("br")) transistor_31 (.in(1'b0), .out(LP5), .gate(transistor_33_out));
  Transistor #(.\type ("n"), .gate("br")) transistor_32 (.in(1'b0), .out(LP6), .gate(transistor_33_out));
  Transistor #(.\type ("n")) transistor_33 (.in(1'b0), .out(transistor_33_out), .gate(not_1_out));
  Transistor #(.\type ("n")) transistor_34 (.in(1'b0), .out(transistor_33_out), .gate(not_2_out));
  Transistor #(.\type ("n")) transistor_35 (.in(1'b0), .out(transistor_33_out), .gate(F1));
  Transistor #(.\type ("n")) transistor_36 (.in(1'b0), .out(transistor_33_out), .gate(not_4_out));
  Pull_Resistor #(.pull(1)) pull_resistor_3 (.node(transistor_33_out));
  Transistor #(.\type ("n"), .gate("br")) transistor_37 (.in(1'b0), .out(LP0), .gate(transistor_62_out));
  Transistor #(.\type ("n"), .gate("br")) transistor_38 (.in(1'b0), .out(LP1), .gate(transistor_62_out));
  Transistor #(.\type ("n"), .gate("br")) transistor_39 (.in(1'b0), .out(LP2), .gate(transistor_52_out));
  Transistor #(.\type ("n"), .gate("br")) transistor_40 (.in(1'b0), .out(LP2), .gate(transistor_62_out));
  Transistor #(.\type ("n"), .gate("br")) transistor_41 (.in(1'b0), .out(LP3), .gate(transistor_52_out));
  Transistor #(.\type ("n"), .gate("br")) transistor_42 (.in(1'b0), .out(LP3), .gate(transistor_62_out));
  Transistor #(.\type ("n"), .gate("br")) transistor_43 (.in(1'b0), .out(LP5), .gate(transistor_52_out));
  Transistor #(.\type ("n"), .gate("br")) transistor_44 (.in(1'b0), .out(LP6), .gate(transistor_52_out));
  Transistor #(.\type ("n"), .gate("br")) transistor_45 (.in(1'b0), .out(LP6), .gate(transistor_62_out));
  Transistor #(.\type ("n"), .gate("br")) transistor_46 (.in(1'b0), .out(LP7), .gate(transistor_52_out));
  Transistor #(.\type ("n"), .gate("br")) transistor_47 (.in(1'b0), .out(LP7), .gate(transistor_62_out));
  Transistor #(.\type ("n"), .gate("br")) transistor_48 (.in(1'b0), .out(LP8), .gate(transistor_52_out));
  Transistor #(.\type ("n"), .gate("br")) transistor_49 (.in(1'b0), .out(LP8), .gate(transistor_62_out));
  Transistor #(.\type ("n"), .gate("br")) transistor_50 (.in(1'b0), .out(LP10), .gate(transistor_62_out));
  Transistor #(.\type ("n"), .gate("br")) transistor_51 (.in(1'b0), .out(LP10), .gate(transistor_52_out));
  Transistor #(.\type ("n")) transistor_52 (.in(1'b0), .out(transistor_52_out), .gate(not_1_out));
  Transistor #(.\type ("n")) transistor_53 (.in(1'b0), .out(transistor_52_out), .gate(not_2_out));
  Transistor #(.\type ("n")) transistor_54 (.in(1'b0), .out(transistor_52_out), .gate(F1));
  Transistor #(.\type ("n")) transistor_55 (.in(1'b0), .out(transistor_52_out), .gate(F0));
  Pull_Resistor #(.pull(1)) pull_resistor_4 (.node(transistor_52_out));
  Transistor #(.\type ("n"), .gate("br")) transistor_56 (.in(1'b0), .out(LP0), .gate(transistor_63_out));
  Transistor #(.\type ("n"), .gate("br")) transistor_57 (.in(1'b0), .out(LP2), .gate(transistor_63_out));
  Transistor #(.\type ("n"), .gate("br")) transistor_58 (.in(1'b0), .out(LP3), .gate(transistor_63_out));
  Transistor #(.\type ("n"), .gate("br")) transistor_59 (.in(1'b0), .out(LP4), .gate(transistor_63_out));
  Transistor #(.\type ("n"), .gate("br")) transistor_60 (.in(1'b0), .out(LP6), .gate(transistor_63_out));
  Transistor #(.\type ("n"), .gate("br")) transistor_61 (.in(1'b0), .out(LP7), .gate(transistor_63_out));
  Transistor #(.\type ("n")) transistor_62 (.in(1'b0), .out(transistor_62_out), .gate(not_1_out));
  Transistor #(.\type ("n")) transistor_63 (.in(1'b0), .out(transistor_63_out), .gate(not_1_out));
  Transistor #(.\type ("n")) transistor_64 (.in(1'b0), .out(transistor_63_out), .gate(F2));
  Transistor #(.\type ("n")) transistor_65 (.in(1'b0), .out(transistor_62_out), .gate(F2));
  Transistor #(.\type ("n")) transistor_66 (.in(1'b0), .out(transistor_63_out), .gate(not_3_out));
  Transistor #(.\type ("n")) transistor_67 (.in(1'b0), .out(transistor_62_out), .gate(not_3_out));
  Transistor #(.\type ("n")) transistor_68 (.in(1'b0), .out(transistor_63_out), .gate(F0));
  Transistor #(.\type ("n")) transistor_69 (.in(1'b0), .out(transistor_62_out), .gate(not_4_out));
  Pull_Resistor #(.pull(1)) pull_resistor_5 (.node(transistor_62_out));
  Pull_Resistor #(.pull(1)) pull_resistor_6 (.node(transistor_63_out));
  Transistor #(.\type ("n"), .gate("br")) transistor_70 (.in(1'b0), .out(LP0), .gate(transistor_78_out));
  Transistor #(.\type ("n"), .gate("br")) transistor_71 (.in(1'b0), .out(LP1), .gate(transistor_78_out));
  Transistor #(.\type ("n"), .gate("br")) transistor_72 (.in(1'b0), .out(LP3), .gate(transistor_78_out));
  Transistor #(.\type ("n"), .gate("br")) transistor_73 (.in(1'b0), .out(LP4), .gate(transistor_78_out));
  Transistor #(.\type ("n"), .gate("br")) transistor_74 (.in(1'b0), .out(LP5), .gate(transistor_78_out));
  Transistor #(.\type ("n"), .gate("br")) transistor_75 (.in(1'b0), .out(LP6), .gate(transistor_78_out));
  Transistor #(.\type ("n"), .gate("br")) transistor_76 (.in(1'b0), .out(LP7), .gate(transistor_78_out));
  Transistor #(.\type ("n"), .gate("br")) transistor_77 (.in(1'b0), .out(LP10), .gate(transistor_78_out));
  Transistor #(.\type ("n")) transistor_78 (.in(1'b0), .out(transistor_78_out), .gate(not_1_out));
  Transistor #(.\type ("n")) transistor_79 (.in(1'b0), .out(transistor_78_out), .gate(F2));
  Transistor #(.\type ("n")) transistor_80 (.in(1'b0), .out(transistor_78_out), .gate(F1));
  Transistor #(.\type ("n")) transistor_81 (.in(1'b0), .out(transistor_78_out), .gate(not_4_out));
  Pull_Resistor #(.pull(1)) pull_resistor_7 (.node(transistor_78_out));
  Transistor #(.\type ("n"), .gate("br")) transistor_82 (.in(1'b0), .out(LP0), .gate(transistor_88_out));
  Transistor #(.\type ("n"), .gate("br")) transistor_83 (.in(1'b0), .out(LP1), .gate(transistor_88_out));
  Transistor #(.\type ("n"), .gate("br")) transistor_84 (.in(1'b0), .out(LP4), .gate(transistor_88_out));
  Transistor #(.\type ("n"), .gate("br")) transistor_85 (.in(1'b0), .out(LP6), .gate(transistor_88_out));
  Transistor #(.\type ("n"), .gate("br")) transistor_86 (.in(1'b0), .out(LP8), .gate(transistor_88_out));
  Transistor #(.\type ("n"), .gate("br")) transistor_87 (.in(1'b0), .out(LP9), .gate(transistor_88_out));
  Transistor #(.\type ("n")) transistor_88 (.in(1'b0), .out(transistor_88_out), .gate(not_1_out));
  Transistor #(.\type ("n")) transistor_89 (.in(1'b0), .out(transistor_88_out), .gate(F2));
  Transistor #(.\type ("n")) transistor_90 (.in(1'b0), .out(transistor_88_out), .gate(F1));
  Transistor #(.\type ("n")) transistor_91 (.in(1'b0), .out(transistor_88_out), .gate(F0));
  Pull_Resistor #(.pull(1)) pull_resistor_8 (.node(transistor_88_out));
  Transistor #(.\type ("n"), .gate("br")) transistor_92 (.in(1'b0), .out(LP0), .gate(transistor_114_out));
  Transistor #(.\type ("n"), .gate("br")) transistor_93 (.in(1'b0), .out(LP0), .gate(transistor_105_out));
  Transistor #(.\type ("n"), .gate("br")) transistor_94 (.in(1'b0), .out(LP1), .gate(transistor_114_out));
  Transistor #(.\type ("n"), .gate("br")) transistor_95 (.in(1'b0), .out(LP1), .gate(transistor_105_out));
  Transistor #(.\type ("n"), .gate("br")) transistor_96 (.in(1'b0), .out(LP2), .gate(transistor_105_out));
  Transistor #(.\type ("n"), .gate("br")) transistor_97 (.in(1'b0), .out(LP2), .gate(transistor_114_out));
  Transistor #(.\type ("n"), .gate("br")) transistor_98 (.in(1'b0), .out(LP3), .gate(transistor_105_out));
  Transistor #(.\type ("n"), .gate("br")) transistor_99 (.in(1'b0), .out(LP3), .gate(transistor_114_out));
  Transistor #(.\type ("n"), .gate("br")) transistor_100 (.in(1'b0), .out(LP6), .gate(transistor_114_out));
  Transistor #(.\type ("n"), .gate("br")) transistor_101 (.in(1'b0), .out(LP6), .gate(transistor_105_out));
  Transistor #(.\type ("n"), .gate("br")) transistor_102 (.in(1'b0), .out(LP7), .gate(transistor_105_out));
  Transistor #(.\type ("n"), .gate("br")) transistor_103 (.in(1'b0), .out(LP7), .gate(transistor_114_out));
  Transistor #(.\type ("n"), .gate("br")) transistor_104 (.in(1'b0), .out(LP8), .gate(transistor_114_out));
  Transistor #(.\type ("n")) transistor_105 (.in(1'b0), .out(transistor_105_out), .gate(F3));
  Transistor #(.\type ("n")) transistor_106 (.in(1'b0), .out(transistor_105_out), .gate(not_2_out));
  Transistor #(.\type ("n")) transistor_107 (.in(1'b0), .out(transistor_105_out), .gate(not_3_out));
  Transistor #(.\type ("n")) transistor_108 (.in(1'b0), .out(transistor_105_out), .gate(not_4_out));
  Pull_Resistor #(.pull(1)) pull_resistor_9 (.node(transistor_105_out));
  Transistor #(.\type ("n"), .gate("br")) transistor_109 (.in(1'b0), .out(LP0), .gate(transistor_115_out));
  Transistor #(.\type ("n"), .gate("br")) transistor_110 (.in(1'b0), .out(LP1), .gate(transistor_115_out));
  Transistor #(.\type ("n"), .gate("br")) transistor_111 (.in(1'b0), .out(LP3), .gate(transistor_115_out));
  Transistor #(.\type ("n"), .gate("br")) transistor_112 (.in(1'b0), .out(LP7), .gate(transistor_115_out));
  Transistor #(.\type ("n"), .gate("br")) transistor_113 (.in(1'b0), .out(LP8), .gate(transistor_115_out));
  Transistor #(.\type ("n")) transistor_114 (.in(1'b0), .out(transistor_114_out), .gate(F3));
  Transistor #(.\type ("n")) transistor_115 (.in(1'b0), .out(transistor_115_out), .gate(F3));
  Transistor #(.\type ("n")) transistor_116 (.in(1'b0), .out(transistor_114_out), .gate(not_2_out));
  Transistor #(.\type ("n")) transistor_117 (.in(1'b0), .out(transistor_115_out), .gate(not_2_out));
  Transistor #(.\type ("n")) transistor_118 (.in(1'b0), .out(transistor_115_out), .gate(F1));
  Transistor #(.\type ("n")) transistor_119 (.in(1'b0), .out(transistor_114_out), .gate(not_3_out));
  Transistor #(.\type ("n")) transistor_120 (.in(1'b0), .out(transistor_114_out), .gate(F0));
  Transistor #(.\type ("n")) transistor_121 (.in(1'b0), .out(transistor_115_out), .gate(not_4_out));
  Pull_Resistor #(.pull(1)) pull_resistor_10 (.node(transistor_115_out));
  Pull_Resistor #(.pull(1)) pull_resistor_11 (.node(transistor_114_out));
  Transistor #(.\type ("n"), .gate("br")) transistor_122 (.in(1'b0), .out(LP0), .gate(transistor_128_out));
  Transistor #(.\type ("n"), .gate("br")) transistor_123 (.in(1'b0), .out(LP1), .gate(transistor_128_out));
  Transistor #(.\type ("n"), .gate("br")) transistor_124 (.in(1'b0), .out(LP3), .gate(transistor_128_out));
  Transistor #(.\type ("n"), .gate("br")) transistor_125 (.in(1'b0), .out(LP4), .gate(transistor_128_out));
  Transistor #(.\type ("n"), .gate("br")) transistor_126 (.in(1'b0), .out(LP8), .gate(transistor_128_out));
  Transistor #(.\type ("n"), .gate("br")) transistor_127 (.in(1'b0), .out(LP9), .gate(transistor_128_out));
  Transistor #(.\type ("n")) transistor_128 (.in(1'b0), .out(transistor_128_out), .gate(F3));
  Transistor #(.\type ("n")) transistor_129 (.in(1'b0), .out(transistor_128_out), .gate(not_2_out));
  Transistor #(.\type ("n")) transistor_130 (.in(1'b0), .out(transistor_128_out), .gate(F1));
  Transistor #(.\type ("n")) transistor_131 (.in(1'b0), .out(transistor_128_out), .gate(F0));
  Pull_Resistor #(.pull(1)) pull_resistor_12 (.node(transistor_128_out));
  Transistor #(.\type ("n"), .gate("br")) transistor_132 (.in(1'b0), .out(LP0), .gate(transistor_143_out));
  Transistor #(.\type ("n"), .gate("br")) transistor_133 (.in(1'b0), .out(LP0), .gate(transistor_157_out));
  Transistor #(.\type ("n"), .gate("br")) transistor_134 (.in(1'b0), .out(LP1), .gate(transistor_157_out));
  Transistor #(.\type ("n"), .gate("br")) transistor_135 (.in(1'b0), .out(LP2), .gate(transistor_143_out));
  Transistor #(.\type ("n"), .gate("br")) transistor_136 (.in(1'b0), .out(LP2), .gate(transistor_157_out));
  Transistor #(.\type ("n"), .gate("br")) transistor_137 (.in(1'b0), .out(LP4), .gate(transistor_157_out));
  Transistor #(.\type ("n"), .gate("br")) transistor_138 (.in(1'b0), .out(LP4), .gate(transistor_143_out));
  Transistor #(.\type ("n"), .gate("br")) transistor_139 (.in(1'b0), .out(LP6), .gate(transistor_157_out));
  Transistor #(.\type ("n"), .gate("br")) transistor_140 (.in(1'b0), .out(LP8), .gate(transistor_157_out));
  Transistor #(.\type ("n"), .gate("br")) transistor_141 (.in(1'b0), .out(LP8), .gate(transistor_143_out));
  Transistor #(.\type ("n"), .gate("br")) transistor_142 (.in(1'b0), .out(LP10), .gate(transistor_157_out));
  Transistor #(.\type ("n")) transistor_143 (.in(1'b0), .out(transistor_143_out), .gate(F3));
  Transistor #(.\type ("n")) transistor_144 (.in(1'b0), .out(transistor_143_out), .gate(F2));
  Transistor #(.\type ("n")) transistor_145 (.in(1'b0), .out(transistor_143_out), .gate(not_3_out));
  Transistor #(.\type ("n")) transistor_146 (.in(1'b0), .out(transistor_143_out), .gate(not_4_out));
  Pull_Resistor #(.pull(1)) pull_resistor_13 (.node(transistor_143_out));
  Transistor #(.\type ("n"), .gate("br")) transistor_147 (.in(1'b0), .out(LP0), .gate(transistor_156_out));
  Transistor #(.\type ("n"), .gate("br")) transistor_148 (.in(1'b0), .out(LP1), .gate(transistor_156_out));
  Transistor #(.\type ("n"), .gate("br")) transistor_149 (.in(1'b0), .out(LP2), .gate(transistor_156_out));
  Transistor #(.\type ("n"), .gate("br")) transistor_150 (.in(1'b0), .out(LP3), .gate(transistor_156_out));
  Transistor #(.\type ("n"), .gate("br")) transistor_151 (.in(1'b0), .out(LP4), .gate(transistor_156_out));
  Transistor #(.\type ("n"), .gate("br")) transistor_152 (.in(1'b0), .out(LP5), .gate(transistor_156_out));
  Transistor #(.\type ("n"), .gate("br")) transistor_153 (.in(1'b0), .out(LP6), .gate(transistor_156_out));
  Transistor #(.\type ("n"), .gate("br")) transistor_154 (.in(1'b0), .out(LP8), .gate(transistor_156_out));
  Transistor #(.\type ("n"), .gate("br")) transistor_155 (.in(1'b0), .out(LP10), .gate(transistor_156_out));
  Transistor #(.\type ("n")) transistor_156 (.in(1'b0), .out(transistor_156_out), .gate(F3));
  Transistor #(.\type ("n")) transistor_157 (.in(1'b0), .out(transistor_157_out), .gate(F3));
  Transistor #(.\type ("n")) transistor_158 (.in(1'b0), .out(transistor_156_out), .gate(F2));
  Transistor #(.\type ("n")) transistor_159 (.in(1'b0), .out(transistor_157_out), .gate(F2));
  Transistor #(.\type ("n")) transistor_160 (.in(1'b0), .out(transistor_156_out), .gate(F1));
  Transistor #(.\type ("n")) transistor_161 (.in(1'b0), .out(transistor_157_out), .gate(not_3_out));
  Transistor #(.\type ("n")) transistor_162 (.in(1'b0), .out(transistor_157_out), .gate(F0));
  Transistor #(.\type ("n")) transistor_163 (.in(1'b0), .out(transistor_156_out), .gate(not_4_out));
  Pull_Resistor #(.pull(1)) pull_resistor_14 (.node(transistor_156_out));
  Pull_Resistor #(.pull(1)) pull_resistor_15 (.node(transistor_157_out));
  Transistor #(.\type ("n"), .gate("br")) transistor_164 (.in(1'b0), .out(LP0), .gate(transistor_174_out));
  Transistor #(.\type ("n"), .gate("br")) transistor_165 (.in(1'b0), .out(LP1), .gate(transistor_174_out));
  Transistor #(.\type ("n"), .gate("br")) transistor_166 (.in(1'b0), .out(LP2), .gate(transistor_174_out));
  Transistor #(.\type ("n"), .gate("br")) transistor_167 (.in(1'b0), .out(LP3), .gate(transistor_174_out));
  Transistor #(.\type ("n"), .gate("br")) transistor_168 (.in(1'b0), .out(LP4), .gate(transistor_174_out));
  Transistor #(.\type ("n"), .gate("br")) transistor_169 (.in(1'b0), .out(LP5), .gate(transistor_174_out));
  Transistor #(.\type ("n"), .gate("br")) transistor_170 (.in(1'b0), .out(LP6), .gate(transistor_174_out));
  Transistor #(.\type ("n"), .gate("br")) transistor_171 (.in(1'b0), .out(LP7), .gate(transistor_174_out));
  Transistor #(.\type ("n"), .gate("br")) transistor_172 (.in(1'b0), .out(LP8), .gate(transistor_174_out));
  Transistor #(.\type ("n"), .gate("br")) transistor_173 (.in(1'b0), .out(LP10), .gate(transistor_174_out));
  Transistor #(.\type ("n")) transistor_174 (.in(1'b0), .out(transistor_174_out), .gate(F3));
  Transistor #(.\type ("n")) transistor_175 (.in(1'b0), .out(transistor_174_out), .gate(F2));
  Transistor #(.\type ("n")) transistor_176 (.in(1'b0), .out(transistor_174_out), .gate(F1));
  Transistor #(.\type ("n")) transistor_177 (.in(1'b0), .out(transistor_174_out), .gate(F0));
  Pull_Resistor #(.pull(1)) pull_resistor_16 (.node(transistor_174_out));
  Pull_Resistor #(.pull(1)) pull_resistor_17 (.node(LP0));
  Pull_Resistor #(.pull(1)) pull_resistor_18 (.node(LP1));
  Pull_Resistor #(.pull(1)) pull_resistor_19 (.node(LP2));
  Pull_Resistor #(.pull(1)) pull_resistor_20 (.node(LP3));
  Pull_Resistor #(.pull(1)) pull_resistor_21 (.node(LP4));
  Pull_Resistor #(.pull(1)) pull_resistor_22 (.node(LP5));
  Pull_Resistor #(.pull(1)) pull_resistor_23 (.node(LP6));
  Pull_Resistor #(.pull(1)) pull_resistor_24 (.node(LP7));
  Pull_Resistor #(.pull(1)) pull_resistor_25 (.node(LP8));
  Pull_Resistor #(.pull(1)) pull_resistor_26 (.node(LP9));
  Pull_Resistor #(.pull(1)) pull_resistor_27 (.node(LP10));
endmodule

// NOISE LFSR
module NOISE_LFSR (
  input  RSTEP,
  input  ACLK,
  input  W400E,
  input  D7,
  input  NORND,
  output RNDOUT
);

  wire and_1_out, and_2_out, dpos_1_q, dpos_2_q, dpos_3_q, dpos_4_q, dpos_5_q, dpos_6_q, dpos_7_q, dpos_8_q,
       dpos_9_q, dpos_10_q, dpos_11_q, dpos_12_q, dpos_13_q, dpos_14_q, dpos_15_q, dpos_16_q,
       multiplexer_1_out, nor_1_out, nor_2_out, nor_3_out, nor_4_out;

  and and_1 (and_1_out, ACLK, W400E);
  Dpos dpos_1 (.Clk(and_1_out), .In(D7), .Q(dpos_1_q));  // open: nQ
  and and_2 (and_2_out, multiplexer_1_out, dpos_16_q);
  nor nor_1 (nor_1_out, multiplexer_1_out, dpos_16_q, nor_4_out);
  nor nor_2 (nor_2_out, nor_1_out, and_2_out);
  Dpos dpos_2 (.Clk(RSTEP), .In(nor_2_out), .Q(dpos_2_q));  // open: nQ
  Dpos dpos_3 (.Clk(RSTEP), .In(dpos_2_q), .Q(dpos_3_q));  // open: nQ
  Dpos dpos_4 (.Clk(RSTEP), .In(dpos_3_q), .Q(dpos_4_q));  // open: nQ
  Dpos dpos_5 (.Clk(RSTEP), .In(dpos_4_q), .Q(dpos_5_q));  // open: nQ
  Dpos dpos_6 (.Clk(RSTEP), .In(dpos_5_q), .Q(dpos_6_q));  // open: nQ
  Dpos dpos_7 (.Clk(RSTEP), .In(dpos_6_q), .Q(dpos_7_q));  // open: nQ
  Dpos dpos_8 (.Clk(RSTEP), .In(dpos_7_q), .Q(dpos_8_q));  // open: nQ
  Dpos dpos_9 (.Clk(RSTEP), .In(dpos_8_q), .Q(dpos_9_q));  // open: nQ
  Dpos dpos_10 (.Clk(RSTEP), .In(dpos_9_q), .Q(dpos_10_q));  // open: nQ
  Dpos dpos_11 (.Clk(RSTEP), .In(dpos_10_q), .Q(dpos_11_q));  // open: nQ
  Dpos dpos_12 (.Clk(RSTEP), .In(dpos_11_q), .Q(dpos_12_q));  // open: nQ
  Dpos dpos_13 (.Clk(RSTEP), .In(dpos_12_q), .Q(dpos_13_q));  // open: nQ
  Dpos dpos_14 (.Clk(RSTEP), .In(dpos_13_q), .Q(dpos_14_q));  // open: nQ
  Dpos dpos_15 (.Clk(RSTEP), .In(dpos_14_q), .Q(dpos_15_q));  // open: nQ
  Dpos dpos_16 (.Clk(RSTEP), .In(dpos_15_q), .Q(dpos_16_q));  // open: nQ
  nor nor_3 (nor_3_out, dpos_16_q, NORND);
  Multiplexer #(.enable("false")) multiplexer_1 (
    .in0(dpos_15_q), .in1(dpos_10_q), .out(multiplexer_1_out), .sel(dpos_1_q));
  not not_1 (RNDOUT, nor_3_out);
  nor nor_4 (nor_4_out, dpos_2_q, dpos_3_q, dpos_4_q, dpos_5_q, dpos_6_q, dpos_7_q, dpos_8_q, dpos_9_q, dpos_10_q, dpos_11_q, dpos_12_q, dpos_13_q, dpos_14_q, dpos_15_q, dpos_16_q);
endmodule

module Dpos (
  input  Clk,
  input  In,
  output Q,
  output nQ
);

  D_Flip_Flop d_ff_1 (.clk(Clk), .D(In), .Q(Q), .Qn(nQ));  // open: preset, en, reset
endmodule

// ENVELOPE FREQUENCY DIVIDER
module NOISE_ENVELOPE_FREQUENCY_DIVIDER (
  input  nACLK,
  input  STEP,
  input  LOAD,
  input  Vol0,
  input  RES,
  input  Vol1,
  input  Vol2,
  input  Vol3,
  output Output
);

  wire and_1_out, and_2_out, and_3_out, and_4_out, and_5_out, and_6_out, and_7_out, and_8_out, d_ff_1_q,
       d_ff_1_qn, d_ff_2_q, d_ff_2_qn, d_ff_3_q, d_ff_3_qn, d_ff_4_q, d_ff_4_qn, d_ff_5_qn, d_ff_6_qn,
       d_ff_7_qn, d_ff_8_qn, multiplexer_1_out, multiplexer_2_out, multiplexer_3_out, multiplexer_4_out,
       nor_1_out, nor_2_out, nor_3_out, not_1_out, not_2_out, not_3_out, not_4_out, not_5_out, not_6_out,
       not_7_out, not_8_out, or_1_out, or_2_out, or_3_out, or_4_out;

  not not_1 (not_1_out, Vol0);
  not not_2 (not_2_out, Vol1);
  not not_3 (not_3_out, Vol2);
  not not_4 (not_4_out, Vol3);
  D_Flip_Flop d_ff_1 (
    .clk(STEP), .D(d_ff_5_qn), .Q(d_ff_1_q), .Qn(d_ff_1_qn), .preset(and_1_out), .reset(or_1_out));  // open: en
  or or_1 (or_1_out, and_2_out, RES);
  and and_1 (and_1_out, LOAD, Vol0);
  and and_2 (and_2_out, LOAD, not_1_out);
  D_Flip_Flop d_ff_2 (
    .clk(STEP), .D(d_ff_6_qn), .Q(d_ff_2_q), .Qn(d_ff_2_qn), .preset(and_3_out), .reset(or_2_out));  // open: en
  or or_2 (or_2_out, and_4_out, RES);
  and and_3 (and_3_out, LOAD, Vol1);
  and and_4 (and_4_out, LOAD, not_2_out);
  D_Flip_Flop d_ff_3 (
    .clk(STEP), .D(d_ff_7_qn), .Q(d_ff_3_q), .Qn(d_ff_3_qn), .preset(and_5_out), .reset(or_3_out));  // open: en
  or or_3 (or_3_out, and_6_out, RES);
  and and_5 (and_5_out, LOAD, Vol2);
  and and_6 (and_6_out, LOAD, not_3_out);
  D_Flip_Flop d_ff_4 (
    .clk(STEP), .D(d_ff_8_qn), .Q(d_ff_4_q), .Qn(d_ff_4_qn), .preset(and_7_out), .reset(or_4_out));  // open: en
  or or_4 (or_4_out, and_8_out, RES);
  and and_7 (and_7_out, LOAD, Vol3);
  and and_8 (and_8_out, LOAD, not_4_out);
  D_Flip_Flop d_ff_5 (.clk(nACLK), .D(multiplexer_1_out), .Qn(d_ff_5_qn));  // open: Q, preset, en, reset
  Multiplexer #(.enable("false")) multiplexer_1 (.in0(d_ff_1_qn), .in1(d_ff_1_q), .out(multiplexer_1_out), .sel(1'b1));
  not not_5 (not_5_out, 1'b1);
  D_Flip_Flop d_ff_6 (.clk(nACLK), .D(multiplexer_2_out), .Qn(d_ff_6_qn));  // open: Q, preset, en, reset
  Multiplexer #(.enable("false")) multiplexer_2 (
    .in0(d_ff_2_qn), .in1(d_ff_2_q), .out(multiplexer_2_out), .sel(nor_1_out));
  not not_6 (not_6_out, nor_1_out);
  D_Flip_Flop d_ff_7 (.clk(nACLK), .D(multiplexer_3_out), .Qn(d_ff_7_qn));  // open: Q, preset, en, reset
  Multiplexer #(.enable("false")) multiplexer_3 (
    .in0(d_ff_3_qn), .in1(d_ff_3_q), .out(multiplexer_3_out), .sel(nor_2_out));
  not not_7 (not_7_out, nor_2_out);
  D_Flip_Flop d_ff_8 (.clk(nACLK), .D(multiplexer_4_out), .Qn(d_ff_8_qn));  // open: Q, preset, en, reset
  Multiplexer #(.enable("false")) multiplexer_4 (
    .in0(d_ff_4_qn), .in1(d_ff_4_q), .out(multiplexer_4_out), .sel(nor_3_out));
  not not_8 (not_8_out, nor_3_out);
  nor nor_1 (nor_1_out, d_ff_1_q, not_5_out);
  nor nor_2 (nor_2_out, d_ff_2_q, not_6_out);
  nor nor_3 (nor_3_out, d_ff_3_q, not_7_out);
  nor nor_4 (Output, d_ff_4_q, not_8_out);
endmodule

// ENVELOPE CONTROL
module NOISE_ENVELOPE_CONTROL (
  input  nACLK,
  input  nLFO1,
  input  W400F,
  input  Input_ERC,
  input  Input_OEC,
  input  RND_LC,
  output RELOAD,
  output LOAD,
  output STEP,
  output Estep,
  output Eres,
  output Output_OEC
);

  wire d_ff_1_q, d_ff_2_qn, d_ff_3_q, d_ff_4_q, d_ff_5_q, d_ff_6_q, nor_1_out, nor_3_out, nor_4_out,
       nor_7_out, not_1_out, not_2_out;

  nor nor_1 (nor_1_out, W400F, RELOAD);
  nor nor_2 (RELOAD, nor_1_out, nor_4_out);
  D_Flip_Flop d_ff_1 (.clk(nACLK), .D(nor_3_out), .Q(d_ff_1_q));  // open: Qn, preset, en, reset
  nor nor_3 (nor_3_out, RELOAD, Input_ERC);
  D_Flip_Flop d_ff_2 (.clk(nACLK), .D(nor_3_out), .Qn(d_ff_2_qn));  // open: Q, preset, en, reset
  D_Flip_Flop d_ff_3 (.clk(nACLK), .D(nor_1_out), .Q(d_ff_3_q));  // open: Qn, preset, en, reset
  nor nor_4 (nor_4_out, nLFO1, d_ff_3_q);
  D_Flip_Flop d_ff_4 (.clk(nACLK), .D(RELOAD), .Q(d_ff_4_q));  // open: Qn, preset, en, reset
  D_Flip_Flop d_ff_5 (.clk(nACLK), .D(Input_OEC), .Q(d_ff_5_q));  // open: Qn, preset, en, reset
  D_Flip_Flop d_ff_6 (.clk(nACLK), .D(Input_OEC), .Q(d_ff_6_q));  // open: Qn, preset, en, reset
  nor nor_5 (LOAD, nLFO1, d_ff_1_q);
  nor nor_6 (STEP, nLFO1, d_ff_2_qn);
  not not_1 (not_1_out, LOAD);
  not not_2 (not_2_out, nor_7_out);
  nor nor_7 (nor_7_out, d_ff_4_q, d_ff_5_q);
  nand nand_1 (Output_OEC, d_ff_6_q, RND_LC);
  nor nor_8 (Estep, not_1_out, not_2_out);
  nor nor_9 (Eres, not_1_out, nor_7_out);

  // Notes on the sheet:
  //   NORFF1
  //   NORFF2
  //   RELOAD
  //   NOR1
  //   NOR6
  //   NOR4
  //   NOR5
  //   INV1
  //   NOR2
  //   NAND
  //   INV2
  //   NOR7
  //   NOR8
endmodule

// ENVELOPE OUTPUT COUNTER
module NOISE_ENVELOPE_OUTPUT_COUNTER (
  input  nACLK,
  input  Input_OEC,
  input  Eres,
  input  Estep,
  input  RES,
  input  Reload,
  output Env0,
  output Env1,
  output Env2,
  output Env3,
  output Output_OEC
);

  wire and_1_out, and_2_out, and_3_out, and_4_out, and_5_out, and_6_out, and_7_out, and_8_out, d_ff_1_qn,
       d_ff_2_qn, d_ff_3_qn, d_ff_4_qn, d_ff_5_qn, d_ff_6_qn, d_ff_7_qn, d_ff_8_qn, multiplexer_1_out,
       multiplexer_2_out, multiplexer_3_out, multiplexer_4_out, nor_1_out, nor_2_out, nor_3_out, not_1_out,
       not_2_out, not_3_out, not_4_out, not_5_out, not_6_out, not_7_out, not_8_out, or_1_out, or_2_out,
       or_3_out, or_4_out;

  and and_1 (and_1_out, Eres, Input_OEC);
  and and_2 (and_2_out, Eres, not_1_out);
  not not_1 (not_1_out, Input_OEC);
  and and_3 (and_3_out, Eres, Input_OEC);
  and and_4 (and_4_out, Eres, not_2_out);
  not not_2 (not_2_out, Input_OEC);
  and and_5 (and_5_out, Eres, Input_OEC);
  and and_6 (and_6_out, Eres, not_3_out);
  not not_3 (not_3_out, Input_OEC);
  and and_7 (and_7_out, Eres, Input_OEC);
  and and_8 (and_8_out, Eres, not_4_out);
  not not_4 (not_4_out, Input_OEC);
  D_Flip_Flop d_ff_1 (
    .clk(Estep), .D(d_ff_5_qn), .Q(Env0), .Qn(d_ff_1_qn), .preset(and_1_out), .reset(or_1_out));  // open: en
  or or_1 (or_1_out, RES, and_2_out);
  D_Flip_Flop d_ff_2 (
    .clk(Estep), .D(d_ff_6_qn), .Q(Env1), .Qn(d_ff_2_qn), .preset(and_3_out), .reset(or_2_out));  // open: en
  or or_2 (or_2_out, RES, and_4_out);
  D_Flip_Flop d_ff_3 (
    .clk(Estep), .D(d_ff_7_qn), .Q(Env2), .Qn(d_ff_3_qn), .preset(and_5_out), .reset(or_3_out));  // open: en
  or or_3 (or_3_out, RES, and_6_out);
  D_Flip_Flop d_ff_4 (
    .clk(Estep), .D(d_ff_8_qn), .Q(Env3), .Qn(d_ff_4_qn), .preset(and_7_out), .reset(or_4_out));  // open: en
  or or_4 (or_4_out, RES, and_8_out);
  Multiplexer #(.enable("false")) multiplexer_1 (.in0(d_ff_1_qn), .in1(Env0), .out(multiplexer_1_out), .sel(1'b1));
  not not_5 (not_5_out, 1'b1);
  Multiplexer #(.enable("false")) multiplexer_2 (.in0(d_ff_2_qn), .in1(Env1), .out(multiplexer_2_out), .sel(nor_1_out));
  not not_6 (not_6_out, nor_1_out);
  Multiplexer #(.enable("false")) multiplexer_3 (.in0(d_ff_3_qn), .in1(Env2), .out(multiplexer_3_out), .sel(nor_2_out));
  not not_7 (not_7_out, nor_2_out);
  Multiplexer #(.enable("false")) multiplexer_4 (.in0(d_ff_4_qn), .in1(Env3), .out(multiplexer_4_out), .sel(nor_3_out));
  not not_8 (not_8_out, nor_3_out);
  D_Flip_Flop d_ff_5 (.clk(nACLK), .D(multiplexer_1_out), .Qn(d_ff_5_qn));  // open: Q, preset, en, reset
  D_Flip_Flop d_ff_6 (.clk(nACLK), .D(multiplexer_2_out), .Qn(d_ff_6_qn));  // open: Q, preset, en, reset
  D_Flip_Flop d_ff_7 (.clk(nACLK), .D(multiplexer_3_out), .Qn(d_ff_7_qn));  // open: Q, preset, en, reset
  D_Flip_Flop d_ff_8 (.clk(nACLK), .D(multiplexer_4_out), .Qn(d_ff_8_qn));  // open: Q, preset, en, reset
  nor nor_1 (nor_1_out, Env0, not_5_out);
  nor nor_2 (nor_2_out, Env1, not_6_out);
  nor nor_3 (nor_3_out, Env2, not_7_out);
  nor nor_4 (Output_OEC, Env3, Reload, not_8_out);
endmodule

// DPCM CHANNEL
module DPCM_CHANNEL (
  input  PHI1,
  input  ACLK,
  input  nACLK,
  input  W4010,
  input  W4011,
  input  W4012,
  input  W4013,
  input  W4015,
  input  nR4015,
  input  D0,
  input  D1,
  input  D2,
  input  D3,
  input  D4,
  input  D5,
  input  D6,
  input  D7,
  input  R_W,
  input  Res,
  output D4_2,
  output nDMCINT,
  output D7_2,
  output RUNDMC,
  output out_24,
  output Z4,
  output DMC0,
  output DMC1,
  output DMC2,
  output DMC3,
  output DMC4,
  output DMC5,
  output DMC6,
  output DMCA0,
  output DMCA1,
  output DMCA2,
  output DMCA3,
  output DMCA4,
  output DMCA5,
  output DMCA6,
  output DMCA7,
  output DMCA8,
  output DMCA9,
  output DMCA10,
  output DMCA11,
  output DMCA12,
  output DMCA13,
  output DMCA14
);

  wire dpcm_control_1_bload, dpcm_control_1_bstep, dpcm_control_1_dstep, dpcm_control_1_nfload,
       dpcm_control_1_nstep, dpcm_control_1_pcm, dpcm_control_1_sload, dpcm_control_1_sstep,
       dpcm_lfsr_frequency_1_fload, dpcm_output_counter_1_dout, dpcm_register_1_d0_2, dpcm_register_1_d1_2,
       dpcm_register_1_d2_2, dpcm_register_1_d3_2, dpcm_register_1_d6_2, dpcm_register_1_nd7,
       dpcm_register_3_d0_2, dpcm_register_3_d1_2, dpcm_register_3_d2_2, dpcm_register_3_d3_2,
       dpcm_register_3_d4_2, dpcm_register_3_d5_2, dpcm_register_3_d6_2, dpcm_register_3_d7_2,
       dpcm_sample_bit_counter_1_nout, dpcm_sample_lenght_counter_1_sout, dpcm_sample_shift_register_1_bout,
       not_1_out;
  wire [7:0] controlled_buffer_1_out, dpcm_register_2_d0_2;

  DPCM_REGISTER dpcm_register_1 (
    .ACLK(ACLK), .W40xx(W4010), .D0(D0), .D1(D1), .D2(D2), .D3(D3), .D4(D4), .D5(D5), .D6(D6), .D7(D7),
    .D0_2(dpcm_register_1_d0_2), .D1_2(dpcm_register_1_d1_2), .D2_2(dpcm_register_1_d2_2),
    .D3_2(dpcm_register_1_d3_2), .D6_2(dpcm_register_1_d6_2), .nD7(dpcm_register_1_nd7));  // open: D4_2, D5_2, D7_2
  DPCM_REGISTER dpcm_register_2 (
    .ACLK(ACLK), .W40xx(W4012), .D0(D0), .D1(D1), .D2(D2), .D3(D3), .D4(D4), .D5(D5), .D6(D6), .D7(D7),
    .D0_2(dpcm_register_2_d0_2[0]), .D1_2(dpcm_register_2_d0_2[1]), .D2_2(dpcm_register_2_d0_2[2]),
    .D3_2(dpcm_register_2_d0_2[3]), .D4_2(dpcm_register_2_d0_2[4]), .D5_2(dpcm_register_2_d0_2[5]),
    .D6_2(dpcm_register_2_d0_2[6]), .D7_2(dpcm_register_2_d0_2[7]));  // open: nD7
  DPCM_REGISTER dpcm_register_3 (
    .ACLK(ACLK), .W40xx(W4013), .D0(D0), .D1(D1), .D2(D2), .D3(D3), .D4(D4), .D5(D5), .D6(D6), .D7(D7),
    .D0_2(dpcm_register_3_d0_2), .D1_2(dpcm_register_3_d1_2), .D2_2(dpcm_register_3_d2_2),
    .D3_2(dpcm_register_3_d3_2), .D4_2(dpcm_register_3_d4_2), .D5_2(dpcm_register_3_d5_2),
    .D6_2(dpcm_register_3_d6_2), .D7_2(dpcm_register_3_d7_2));  // open: nD7
  not not_1 (not_1_out, ACLK);
  DPCM_LFSR_FREQUENCY dpcm_lfsr_frequency_1 (
    .nACLK(nACLK), .nACLK2(not_1_out), .Res(Res), .F0(dpcm_register_1_d0_2), .F1(dpcm_register_1_d1_2),
    .F2(dpcm_register_1_d2_2), .F3(dpcm_register_1_d3_2), .FLOAD(dpcm_lfsr_frequency_1_fload));  // open: FSTEP
  DPCM_SAMPLE_BIT_COUNTER dpcm_sample_bit_counter_1 (
    .nACLK(nACLK), .RES(dpcm_control_1_nstep), .NSTEP(Res), .NOUT(dpcm_sample_bit_counter_1_nout));
  DPCM_CONTROL dpcm_control_1 (
    .ACLK(ACLK), .nACLK(nACLK), .PHI1(PHI1), .D4(D4), .W4015(W4015), .nR4015(nR4015),
    .ENIRQ(dpcm_register_1_nd7), .Res(Res), .LOOP(dpcm_register_1_d6_2),
    .SOUT(dpcm_sample_lenght_counter_1_sout), .R_W(R_W), .FLOAD(dpcm_lfsr_frequency_1_fload),
    .DOUT(dpcm_output_counter_1_dout), .NOUT(dpcm_sample_bit_counter_1_nout), .D4_2(D4_2), .nDMCINT(nDMCINT),
    .D7(D7_2), .SSTEP(dpcm_control_1_sstep), .SLOAD(dpcm_control_1_sload), .RUNDMC(RUNDMC), .out_21(out_24),
    .Z4(Z4), .NSTEP(dpcm_control_1_nstep), .nFLOAD(dpcm_control_1_nfload), .DSTEP(dpcm_control_1_dstep),
    .PCM(dpcm_control_1_pcm), .BLOAD(dpcm_control_1_bload), .BSTEP(dpcm_control_1_bstep));
  DPCM_SAMPLE_LENGHT_COUNTER dpcm_sample_lenght_counter_1 (
    .nACLK(nACLK), .SLOAD(dpcm_control_1_sload), .SSTEP(dpcm_control_1_sstep), .RES(Res),
    .LSC0(dpcm_register_3_d0_2), .LSC1(dpcm_register_3_d1_2), .LSC2(dpcm_register_3_d2_2),
    .LSC3(dpcm_register_3_d3_2), .LSC4(dpcm_register_3_d4_2), .LSC5(dpcm_register_3_d5_2),
    .LSC6(dpcm_register_3_d6_2), .LSC7(dpcm_register_3_d7_2), .SOUT(dpcm_sample_lenght_counter_1_sout));
  DPCM_ADDRESS_COUNTER dpcm_address_counter_1 (
    .nACLK(nACLK), .SLOAD(dpcm_control_1_sload), .SSTEP(dpcm_control_1_sstep), .RES(Res),
    .LDMC6(dpcm_register_2_d0_2[0]), .LDMC7(dpcm_register_2_d0_2[1]), .LDMC8(dpcm_register_2_d0_2[2]),
    .LDMC9(dpcm_register_2_d0_2[3]), .LDMC10(dpcm_register_2_d0_2[4]), .LDMC11(dpcm_register_2_d0_2[5]),
    .LDMC12(dpcm_register_2_d0_2[6]), .LDMC13(dpcm_register_2_d0_2[7]), .DMC_A0(DMCA0), .DMC_A1(DMCA1),
    .DMC_A2(DMCA2), .DMC_A3(DMCA3), .DMC_A4(DMCA4), .DMC_A5(DMCA5), .DMC_A6(DMCA6), .DMC_A7(DMCA7),
    .DMC_A8(DMCA8), .DMC_A9(DMCA9), .DMC_A10(DMCA10), .DMC_A11(DMCA11), .DMC_A12(DMCA12), .DMC_A13(DMCA13),
    .DMC_A14(DMCA14));
  assign controlled_buffer_1_out = W4011 ? {D7, D6, D5, D4, D3, D2, D1, D0} : 8'bz;  // Controlled_Buffer controlled_buffer_1
  DPCM_OUTPUT_COUNTER dpcm_output_counter_1 (
    .nACLK(nACLK), .ACLK(ACLK), .W4011(W4011), .DSTEP(dpcm_control_1_dstep), .RES(Res),
    .BOUT(dpcm_sample_shift_register_1_bout), .DL0(controlled_buffer_1_out[0]),
    .DL1(controlled_buffer_1_out[1]), .DL2(controlled_buffer_1_out[2]), .DL3(controlled_buffer_1_out[3]),
    .DL4(controlled_buffer_1_out[4]), .DL5(controlled_buffer_1_out[5]), .DL6(controlled_buffer_1_out[6]),
    .DMC0(DMC0), .DMC1(DMC1), .DMC2(DMC2), .DMC3(DMC3), .DMC4(DMC4), .DMC5(DMC5), .DMC6(DMC6),
    .DOUT(dpcm_output_counter_1_dout));
  DPCM_SAMPLE_SHIFT_REGISTER dpcm_sample_shift_register_1 (
    .ACLK(1'b0), .nACLK(nACLK), .SL0(controlled_buffer_1_out[0]), .SL1(controlled_buffer_1_out[1]),
    .SL2(controlled_buffer_1_out[2]), .SL3(controlled_buffer_1_out[3]), .SL4(controlled_buffer_1_out[4]),
    .SL5(controlled_buffer_1_out[5]), .SL6(controlled_buffer_1_out[6]), .SL7(controlled_buffer_1_out[7]),
    .BSTEP(dpcm_control_1_bstep), .BLOAD(dpcm_control_1_bload), .res(Res), .PCM(dpcm_control_1_pcm),
    .BOUT(dpcm_sample_shift_register_1_bout));
endmodule

module DPCM_REGISTER (
  input  ACLK,
  input  W40xx,
  input  D0,
  input  D1,
  input  D2,
  input  D3,
  input  D4,
  input  D5,
  input  D6,
  input  D7,
  output D0_2,
  output D1_2,
  output D2_2,
  output D3_2,
  output D4_2,
  output D5_2,
  output D6_2,
  output D7_2,
  output nD7
);

  wire and_1_out;

  and and_1 (and_1_out, ACLK, W40xx);
  D_latch d_latch_1 (.EN(and_1_out), .D(D0), .Q(D0_2));  // open: NOT_Q
  D_latch d_latch_2 (.EN(and_1_out), .D(D1), .Q(D1_2));  // open: NOT_Q
  D_latch d_latch_3 (.EN(and_1_out), .D(D2), .Q(D2_2));  // open: NOT_Q
  D_latch d_latch_4 (.EN(and_1_out), .D(D3), .Q(D3_2));  // open: NOT_Q
  D_latch d_latch_5 (.EN(and_1_out), .D(D4), .Q(D4_2));  // open: NOT_Q
  D_latch d_latch_6 (.EN(and_1_out), .D(D5), .Q(D5_2));  // open: NOT_Q
  D_latch d_latch_7 (.EN(and_1_out), .D(D6), .Q(D6_2));  // open: NOT_Q
  D_latch d_latch_8 (.EN(and_1_out), .D(D7), .Q(D7_2), .NOT_Q(nD7));
endmodule

// LFSR FREQUENCY
module DPCM_LFSR_FREQUENCY (
  input  nACLK,
  input  nACLK2,
  input  Res,
  input  F0,
  input  F1,
  input  F2,
  input  F3,
  output FSTEP,
  output FLOAD
);

  wire and_1_out, and_2_out, and_3_out, and_4_out, and_5_out, and_6_out, and_7_out, and_8_out, and_9_out,
       and_10_out, and_11_out, and_12_out, and_13_out, and_14_out, and_15_out, and_16_out, and_17_out,
       and_18_out, and_19_out, d_ff_1_qn, d_ff_2_qn, d_ff_3_qn, d_ff_4_qn, d_ff_5_qn, d_ff_6_qn, d_ff_7_qn,
       d_ff_8_qn, d_ff_9_qn, d_ff_10_qn, d_ff_11_qn, d_ff_12_qn, d_ff_13_qn, d_ff_14_qn, d_ff_15_qn,
       d_ff_16_qn, d_ff_17_qn, d_ff_18_qn, dpcm_table_1_lp0, dpcm_table_1_lp1, dpcm_table_1_lp2,
       dpcm_table_1_lp3, dpcm_table_1_lp4, dpcm_table_1_lp5, dpcm_table_1_lp6, dpcm_table_1_lp7,
       dpcm_table_1_lp8, nor_3_out, nor_4_out, nor_5_out, nor_6_out, nor_7_out, not_1_out, not_2_out,
       not_3_out, not_4_out, not_5_out, not_6_out, not_7_out, not_8_out, not_9_out, not_10_out, not_11_out,
       not_12_out, not_13_out;

  DPCM_TABLE dpcm_table_1 (
    .LP0(dpcm_table_1_lp0), .LP1(dpcm_table_1_lp1), .LP2(dpcm_table_1_lp2), .LP3(dpcm_table_1_lp3),
    .LP4(dpcm_table_1_lp4), .LP5(dpcm_table_1_lp5), .LP6(dpcm_table_1_lp6), .LP7(dpcm_table_1_lp7),
    .LP8(dpcm_table_1_lp8), .F3(F3), .F2(F2), .F1(F1), .F0(F0));
  not not_1 (not_1_out, nACLK2);
  nor nor_1 (FSTEP, not_1_out, nor_5_out);
  nor nor_2 (FLOAD, not_1_out, not_11_out);
  nor nor_3 (nor_3_out, nor_6_out, d_ff_14_qn, d_ff_18_qn);
  and and_1 (and_1_out, d_ff_14_qn, d_ff_18_qn);
  not not_2 (not_2_out, dpcm_table_1_lp0);
  not not_3 (not_3_out, dpcm_table_1_lp1);
  not not_4 (not_4_out, dpcm_table_1_lp2);
  not not_5 (not_5_out, dpcm_table_1_lp3);
  not not_6 (not_6_out, dpcm_table_1_lp4);
  not not_7 (not_7_out, dpcm_table_1_lp5);
  not not_8 (not_8_out, dpcm_table_1_lp6);
  not not_9 (not_9_out, dpcm_table_1_lp7);
  not not_10 (not_10_out, dpcm_table_1_lp8);
  nor nor_4 (nor_4_out, nor_3_out, Res, and_1_out);
  and and_2 (and_2_out, FLOAD, dpcm_table_1_lp0);
  and and_3 (and_3_out, FLOAD, not_2_out);
  and and_4 (and_4_out, FLOAD, dpcm_table_1_lp1);
  and and_5 (and_5_out, FLOAD, not_3_out);
  and and_6 (and_6_out, FLOAD, dpcm_table_1_lp2);
  and and_7 (and_7_out, FLOAD, not_4_out);
  and and_8 (and_8_out, FLOAD, dpcm_table_1_lp3);
  and and_9 (and_9_out, FLOAD, not_5_out);
  and and_10 (and_10_out, FLOAD, dpcm_table_1_lp4);
  and and_11 (and_11_out, FLOAD, not_6_out);
  and and_12 (and_12_out, FLOAD, dpcm_table_1_lp5);
  and and_13 (and_13_out, FLOAD, not_7_out);
  and and_14 (and_14_out, FLOAD, dpcm_table_1_lp6);
  and and_15 (and_15_out, FLOAD, not_8_out);
  and and_16 (and_16_out, FLOAD, dpcm_table_1_lp7);
  and and_17 (and_17_out, FLOAD, not_9_out);
  and and_18 (and_18_out, FLOAD, dpcm_table_1_lp8);
  and and_19 (and_19_out, FLOAD, not_10_out);
  not not_11 (not_11_out, nor_5_out);
  D_Flip_Flop d_ff_1 (
    .clk(FSTEP), .D(nor_4_out), .Qn(d_ff_1_qn), .preset(and_2_out), .reset(and_3_out));  // open: Q, en
  D_Flip_Flop d_ff_2 (
    .clk(FSTEP), .D(d_ff_10_qn), .Qn(d_ff_2_qn), .preset(and_4_out), .reset(and_5_out));  // open: Q, en
  D_Flip_Flop d_ff_3 (
    .clk(FSTEP), .D(d_ff_11_qn), .Qn(d_ff_3_qn), .preset(and_6_out), .reset(and_7_out));  // open: Q, en
  D_Flip_Flop d_ff_4 (
    .clk(FSTEP), .D(d_ff_12_qn), .Qn(d_ff_4_qn), .preset(and_8_out), .reset(and_9_out));  // open: Q, en
  D_Flip_Flop d_ff_5 (
    .clk(FSTEP), .D(d_ff_13_qn), .Qn(d_ff_5_qn), .preset(and_10_out), .reset(and_11_out));  // open: Q, en
  D_Flip_Flop d_ff_6 (
    .clk(FSTEP), .D(d_ff_14_qn), .Qn(d_ff_6_qn), .preset(and_12_out), .reset(and_13_out));  // open: Q, en
  D_Flip_Flop d_ff_7 (
    .clk(FSTEP), .D(d_ff_15_qn), .Qn(d_ff_7_qn), .preset(and_14_out), .reset(and_15_out));  // open: Q, en
  D_Flip_Flop d_ff_8 (
    .clk(FSTEP), .D(d_ff_16_qn), .Qn(d_ff_8_qn), .preset(and_16_out), .reset(and_17_out));  // open: Q, en
  D_Flip_Flop d_ff_9 (
    .clk(FSTEP), .D(d_ff_17_qn), .Qn(d_ff_9_qn), .preset(and_18_out), .reset(and_19_out));  // open: Q, en
  D_Flip_Flop d_ff_10 (.clk(nACLK), .D(d_ff_1_qn), .Qn(d_ff_10_qn));  // open: Q, preset, en, reset
  D_Flip_Flop d_ff_11 (.clk(nACLK), .D(d_ff_2_qn), .Qn(d_ff_11_qn));  // open: Q, preset, en, reset
  D_Flip_Flop d_ff_12 (.clk(nACLK), .D(d_ff_3_qn), .Qn(d_ff_12_qn));  // open: Q, preset, en, reset
  D_Flip_Flop d_ff_13 (.clk(nACLK), .D(d_ff_4_qn), .Qn(d_ff_13_qn));  // open: Q, preset, en, reset
  D_Flip_Flop d_ff_14 (.clk(nACLK), .D(d_ff_5_qn), .Qn(d_ff_14_qn));  // open: Q, preset, en, reset
  D_Flip_Flop d_ff_15 (.clk(nACLK), .D(d_ff_6_qn), .Qn(d_ff_15_qn));  // open: Q, preset, en, reset
  D_Flip_Flop d_ff_16 (.clk(nACLK), .D(d_ff_7_qn), .Qn(d_ff_16_qn));  // open: Q, preset, en, reset
  D_Flip_Flop d_ff_17 (.clk(nACLK), .D(d_ff_8_qn), .Qn(d_ff_17_qn));  // open: Q, preset, en, reset
  D_Flip_Flop d_ff_18 (.clk(nACLK), .D(d_ff_9_qn), .Qn(d_ff_18_qn));  // open: Q, preset, en, reset
  not not_12 (not_12_out, d_ff_18_qn);
  nor nor_5 (nor_5_out, not_13_out, Res);
  nor nor_6 (nor_6_out, d_ff_10_qn, d_ff_11_qn, d_ff_12_qn, d_ff_13_qn, d_ff_14_qn, d_ff_15_qn, d_ff_16_qn, d_ff_17_qn, d_ff_18_qn);
  nor nor_7 (nor_7_out, d_ff_10_qn, d_ff_11_qn, d_ff_12_qn, d_ff_13_qn, d_ff_14_qn, d_ff_15_qn, d_ff_16_qn, d_ff_17_qn, not_12_out);
  not not_13 (not_13_out, nor_7_out);

  // Notes on the sheet:
  //   NOR1
  //   NOR2
  //   NOR3
  //   INV3
endmodule

module DPCM_TABLE (
  input  F3,
  input  F2,
  input  F1,
  input  F0,
  output LP0,
  output LP1,
  output LP2,
  output LP3,
  output LP4,
  output LP5,
  output LP6,
  output LP7,
  output LP8
);

  wire not_1_out, not_2_out, not_3_out, not_4_out, transistor_9_out, transistor_18_out, transistor_19_out,
       transistor_31_out, transistor_42_out, transistor_50_out, transistor_51_out, transistor_65_out,
       transistor_73_out, transistor_83_out, transistor_89_out, transistor_90_out, transistor_100_out,
       transistor_115_out, transistor_122_out, transistor_123_out;

  not not_1 (not_1_out, F3);
  not not_2 (not_2_out, F2);
  not not_3 (not_3_out, F1);
  not not_4 (not_4_out, F0);
  Transistor #(.\type ("n"), .gate("br")) transistor_1 (.in(1'b0), .out(LP1), .gate(transistor_9_out));
  Transistor #(.\type ("n"), .gate("br")) transistor_2 (.in(1'b0), .out(LP2), .gate(transistor_18_out));
  Transistor #(.\type ("n"), .gate("br")) transistor_3 (.in(1'b0), .out(LP3), .gate(transistor_9_out));
  Transistor #(.\type ("n"), .gate("br")) transistor_4 (.in(1'b0), .out(LP3), .gate(transistor_18_out));
  Transistor #(.\type ("n"), .gate("br")) transistor_5 (.in(1'b0), .out(LP4), .gate(transistor_18_out));
  Transistor #(.\type ("n"), .gate("br")) transistor_6 (.in(1'b0), .out(LP5), .gate(transistor_9_out));
  Transistor #(.\type ("n"), .gate("br")) transistor_7 (.in(1'b0), .out(LP8), .gate(transistor_9_out));
  Transistor #(.\type ("n"), .gate("br")) transistor_8 (.in(1'b0), .out(LP8), .gate(transistor_18_out));
  Transistor #(.\type ("n")) transistor_9 (.in(1'b0), .out(transistor_9_out), .gate(not_1_out));
  Transistor #(.\type ("n")) transistor_10 (.in(1'b0), .out(transistor_9_out), .gate(not_2_out));
  Transistor #(.\type ("n")) transistor_11 (.in(1'b0), .out(transistor_9_out), .gate(not_3_out));
  Transistor #(.\type ("n")) transistor_12 (.in(1'b0), .out(transistor_9_out), .gate(not_4_out));
  Pull_Resistor #(.pull(1)) pull_resistor_1 (.node(transistor_9_out));
  Transistor #(.\type ("n"), .gate("br")) transistor_13 (.in(1'b0), .out(LP2), .gate(transistor_19_out));
  Transistor #(.\type ("n"), .gate("br")) transistor_14 (.in(1'b0), .out(LP3), .gate(transistor_19_out));
  Transistor #(.\type ("n"), .gate("br")) transistor_15 (.in(1'b0), .out(LP4), .gate(transistor_19_out));
  Transistor #(.\type ("n"), .gate("br")) transistor_16 (.in(1'b0), .out(LP6), .gate(transistor_19_out));
  Transistor #(.\type ("n"), .gate("br")) transistor_17 (.in(1'b0), .out(LP7), .gate(transistor_19_out));
  Transistor #(.\type ("n")) transistor_18 (.in(1'b0), .out(transistor_18_out), .gate(not_1_out));
  Transistor #(.\type ("n")) transistor_19 (.in(1'b0), .out(transistor_19_out), .gate(not_1_out));
  Transistor #(.\type ("n")) transistor_20 (.in(1'b0), .out(transistor_19_out), .gate(not_2_out));
  Transistor #(.\type ("n")) transistor_21 (.in(1'b0), .out(transistor_18_out), .gate(not_2_out));
  Transistor #(.\type ("n")) transistor_22 (.in(1'b0), .out(transistor_19_out), .gate(F1));
  Transistor #(.\type ("n")) transistor_23 (.in(1'b0), .out(transistor_18_out), .gate(not_3_out));
  Transistor #(.\type ("n")) transistor_24 (.in(1'b0), .out(transistor_18_out), .gate(F0));
  Transistor #(.\type ("n")) transistor_25 (.in(1'b0), .out(transistor_19_out), .gate(not_4_out));
  Pull_Resistor #(.pull(1)) pull_resistor_2 (.node(transistor_19_out));
  Pull_Resistor #(.pull(1)) pull_resistor_3 (.node(transistor_18_out));
  Transistor #(.\type ("n"), .gate("br")) transistor_26 (.in(1'b0), .out(LP0), .gate(transistor_31_out));
  Transistor #(.\type ("n"), .gate("br")) transistor_27 (.in(1'b0), .out(LP2), .gate(transistor_31_out));
  Transistor #(.\type ("n"), .gate("br")) transistor_28 (.in(1'b0), .out(LP3), .gate(transistor_31_out));
  Transistor #(.\type ("n"), .gate("br")) transistor_29 (.in(1'b0), .out(LP4), .gate(transistor_31_out));
  Transistor #(.\type ("n"), .gate("br")) transistor_30 (.in(1'b0), .out(LP7), .gate(transistor_31_out));
  Transistor #(.\type ("n")) transistor_31 (.in(1'b0), .out(transistor_31_out), .gate(not_1_out));
  Transistor #(.\type ("n")) transistor_32 (.in(1'b0), .out(transistor_31_out), .gate(not_2_out));
  Transistor #(.\type ("n")) transistor_33 (.in(1'b0), .out(transistor_31_out), .gate(F1));
  Transistor #(.\type ("n")) transistor_34 (.in(1'b0), .out(transistor_31_out), .gate(F0));
  Pull_Resistor #(.pull(1)) pull_resistor_4 (.node(transistor_31_out));
  Transistor #(.\type ("n"), .gate("br")) transistor_35 (.in(1'b0), .out(LP0), .gate(transistor_42_out));
  Transistor #(.\type ("n"), .gate("br")) transistor_36 (.in(1'b0), .out(LP0), .gate(transistor_50_out));
  Transistor #(.\type ("n"), .gate("br")) transistor_37 (.in(1'b0), .out(LP5), .gate(transistor_50_out));
  Transistor #(.\type ("n"), .gate("br")) transistor_38 (.in(1'b0), .out(LP6), .gate(transistor_50_out));
  Transistor #(.\type ("n"), .gate("br")) transistor_39 (.in(1'b0), .out(LP6), .gate(transistor_42_out));
  Transistor #(.\type ("n"), .gate("br")) transistor_40 (.in(1'b0), .out(LP7), .gate(transistor_50_out));
  Transistor #(.\type ("n"), .gate("br")) transistor_41 (.in(1'b0), .out(LP7), .gate(transistor_42_out));
  Transistor #(.\type ("n")) transistor_42 (.in(1'b0), .out(transistor_42_out), .gate(not_1_out));
  Transistor #(.\type ("n")) transistor_43 (.in(1'b0), .out(transistor_42_out), .gate(F2));
  Transistor #(.\type ("n")) transistor_44 (.in(1'b0), .out(transistor_42_out), .gate(not_3_out));
  Transistor #(.\type ("n")) transistor_45 (.in(1'b0), .out(transistor_42_out), .gate(not_4_out));
  Pull_Resistor #(.pull(1)) pull_resistor_5 (.node(transistor_42_out));
  Transistor #(.\type ("n"), .gate("br")) transistor_46 (.in(1'b0), .out(LP0), .gate(transistor_51_out));
  Transistor #(.\type ("n"), .gate("br")) transistor_47 (.in(1'b0), .out(LP3), .gate(transistor_51_out));
  Transistor #(.\type ("n"), .gate("br")) transistor_48 (.in(1'b0), .out(LP7), .gate(transistor_51_out));
  Transistor #(.\type ("n"), .gate("br")) transistor_49 (.in(1'b0), .out(LP8), .gate(transistor_51_out));
  Transistor #(.\type ("n")) transistor_50 (.in(1'b0), .out(transistor_50_out), .gate(not_1_out));
  Transistor #(.\type ("n")) transistor_51 (.in(1'b0), .out(transistor_51_out), .gate(not_1_out));
  Transistor #(.\type ("n")) transistor_52 (.in(1'b0), .out(transistor_51_out), .gate(F2));
  Transistor #(.\type ("n")) transistor_53 (.in(1'b0), .out(transistor_50_out), .gate(F2));
  Transistor #(.\type ("n")) transistor_54 (.in(1'b0), .out(transistor_51_out), .gate(F1));
  Transistor #(.\type ("n")) transistor_55 (.in(1'b0), .out(transistor_50_out), .gate(not_3_out));
  Transistor #(.\type ("n")) transistor_56 (.in(1'b0), .out(transistor_50_out), .gate(F0));
  Transistor #(.\type ("n")) transistor_57 (.in(1'b0), .out(transistor_51_out), .gate(not_4_out));
  Pull_Resistor #(.pull(1)) pull_resistor_6 (.node(transistor_50_out));
  Pull_Resistor #(.pull(1)) pull_resistor_7 (.node(transistor_51_out));
  Transistor #(.\type ("n"), .gate("br")) transistor_58 (.in(1'b0), .out(LP0), .gate(transistor_65_out));
  Transistor #(.\type ("n"), .gate("br")) transistor_59 (.in(1'b0), .out(LP1), .gate(transistor_65_out));
  Transistor #(.\type ("n"), .gate("br")) transistor_60 (.in(1'b0), .out(LP2), .gate(transistor_65_out));
  Transistor #(.\type ("n"), .gate("br")) transistor_61 (.in(1'b0), .out(LP3), .gate(transistor_65_out));
  Transistor #(.\type ("n"), .gate("br")) transistor_62 (.in(1'b0), .out(LP4), .gate(transistor_65_out));
  Transistor #(.\type ("n"), .gate("br")) transistor_63 (.in(1'b0), .out(LP6), .gate(transistor_65_out));
  Transistor #(.\type ("n"), .gate("br")) transistor_64 (.in(1'b0), .out(LP7), .gate(transistor_65_out));
  Transistor #(.\type ("n")) transistor_65 (.in(1'b0), .out(transistor_65_out), .gate(not_1_out));
  Transistor #(.\type ("n")) transistor_66 (.in(1'b0), .out(transistor_65_out), .gate(F2));
  Transistor #(.\type ("n")) transistor_67 (.in(1'b0), .out(transistor_65_out), .gate(F1));
  Transistor #(.\type ("n")) transistor_68 (.in(1'b0), .out(transistor_65_out), .gate(F0));
  Pull_Resistor #(.pull(1)) pull_resistor_8 (.node(transistor_65_out));
  Transistor #(.\type ("n"), .gate("br")) transistor_69 (.in(1'b0), .out(LP3), .gate(transistor_73_out));
  Transistor #(.\type ("n"), .gate("br")) transistor_70 (.in(1'b0), .out(LP5), .gate(transistor_73_out));
  Transistor #(.\type ("n"), .gate("br")) transistor_71 (.in(1'b0), .out(LP6), .gate(transistor_73_out));
  Transistor #(.\type ("n"), .gate("br")) transistor_72 (.in(1'b0), .out(LP7), .gate(transistor_73_out));
  Transistor #(.\type ("n")) transistor_73 (.in(1'b0), .out(transistor_73_out), .gate(F3));
  Transistor #(.\type ("n")) transistor_74 (.in(1'b0), .out(transistor_73_out), .gate(not_2_out));
  Transistor #(.\type ("n")) transistor_75 (.in(1'b0), .out(transistor_73_out), .gate(not_3_out));
  Transistor #(.\type ("n")) transistor_76 (.in(1'b0), .out(transistor_73_out), .gate(not_4_out));
  Pull_Resistor #(.pull(1)) pull_resistor_9 (.node(transistor_73_out));
  Transistor #(.\type ("n"), .gate("br")) transistor_77 (.in(1'b0), .out(LP0), .gate(transistor_89_out));
  Transistor #(.\type ("n"), .gate("br")) transistor_78 (.in(1'b0), .out(LP0), .gate(transistor_83_out));
  Transistor #(.\type ("n"), .gate("br")) transistor_79 (.in(1'b0), .out(LP1), .gate(transistor_89_out));
  Transistor #(.\type ("n"), .gate("br")) transistor_80 (.in(1'b0), .out(LP1), .gate(transistor_83_out));
  Transistor #(.\type ("n"), .gate("br")) transistor_81 (.in(1'b0), .out(LP2), .gate(transistor_89_out));
  Transistor #(.\type ("n"), .gate("br")) transistor_82 (.in(1'b0), .out(LP7), .gate(transistor_83_out));
  Transistor #(.\type ("n")) transistor_83 (.in(1'b0), .out(transistor_83_out), .gate(F3));
  Transistor #(.\type ("n")) transistor_84 (.in(1'b0), .out(transistor_83_out), .gate(not_2_out));
  Transistor #(.\type ("n")) transistor_85 (.in(1'b0), .out(transistor_83_out), .gate(not_3_out));
  Transistor #(.\type ("n")) transistor_86 (.in(1'b0), .out(transistor_83_out), .gate(F0));
  Pull_Resistor #(.pull(1)) pull_resistor_10 (.node(transistor_83_out));
  Transistor #(.\type ("n"), .gate("br")) transistor_87 (.in(1'b0), .out(LP4), .gate(transistor_90_out));
  Transistor #(.\type ("n"), .gate("br")) transistor_88 (.in(1'b0), .out(LP8), .gate(transistor_90_out));
  Transistor #(.\type ("n")) transistor_89 (.in(1'b0), .out(transistor_89_out), .gate(F3));
  Transistor #(.\type ("n")) transistor_90 (.in(1'b0), .out(transistor_90_out), .gate(F3));
  Transistor #(.\type ("n")) transistor_91 (.in(1'b0), .out(transistor_90_out), .gate(not_2_out));
  Transistor #(.\type ("n")) transistor_92 (.in(1'b0), .out(transistor_89_out), .gate(not_2_out));
  Transistor #(.\type ("n")) transistor_93 (.in(1'b0), .out(transistor_89_out), .gate(F1));
  Transistor #(.\type ("n")) transistor_94 (.in(1'b0), .out(transistor_90_out), .gate(F1));
  Transistor #(.\type ("n")) transistor_95 (.in(1'b0), .out(transistor_90_out), .gate(F0));
  Transistor #(.\type ("n")) transistor_96 (.in(1'b0), .out(transistor_89_out), .gate(not_4_out));
  Pull_Resistor #(.pull(1)) pull_resistor_11 (.node(transistor_90_out));
  Pull_Resistor #(.pull(1)) pull_resistor_12 (.node(transistor_89_out));
  Transistor #(.\type ("n"), .gate("br")) transistor_97 (.in(1'b0), .out(LP0), .gate(transistor_100_out));
  Transistor #(.\type ("n"), .gate("br")) transistor_98 (.in(1'b0), .out(LP3), .gate(transistor_100_out));
  Transistor #(.\type ("n"), .gate("br")) transistor_99 (.in(1'b0), .out(LP6), .gate(transistor_100_out));
  Transistor #(.\type ("n")) transistor_100 (.in(1'b0), .out(transistor_100_out), .gate(F3));
  Transistor #(.\type ("n")) transistor_101 (.in(1'b0), .out(transistor_100_out), .gate(F2));
  Transistor #(.\type ("n")) transistor_102 (.in(1'b0), .out(transistor_100_out), .gate(not_3_out));
  Transistor #(.\type ("n")) transistor_103 (.in(1'b0), .out(transistor_100_out), .gate(not_4_out));
  Pull_Resistor #(.pull(1)) pull_resistor_13 (.node(transistor_100_out));
  Transistor #(.\type ("n"), .gate("br")) transistor_104 (.in(1'b0), .out(LP0), .gate(transistor_122_out));
  Transistor #(.\type ("n"), .gate("br")) transistor_105 (.in(1'b0), .out(LP1), .gate(transistor_115_out));
  Transistor #(.\type ("n"), .gate("br")) transistor_106 (.in(1'b0), .out(LP2), .gate(transistor_122_out));
  Transistor #(.\type ("n"), .gate("br")) transistor_107 (.in(1'b0), .out(LP3), .gate(transistor_122_out));
  Transistor #(.\type ("n"), .gate("br")) transistor_108 (.in(1'b0), .out(LP3), .gate(transistor_115_out));
  Transistor #(.\type ("n"), .gate("br")) transistor_109 (.in(1'b0), .out(LP4), .gate(transistor_115_out));
  Transistor #(.\type ("n"), .gate("br")) transistor_110 (.in(1'b0), .out(LP4), .gate(transistor_122_out));
  Transistor #(.\type ("n"), .gate("br")) transistor_111 (.in(1'b0), .out(LP5), .gate(transistor_115_out));
  Transistor #(.\type ("n"), .gate("br")) transistor_112 (.in(1'b0), .out(LP6), .gate(transistor_115_out));
  Transistor #(.\type ("n"), .gate("br")) transistor_113 (.in(1'b0), .out(LP6), .gate(transistor_122_out));
  Transistor #(.\type ("n"), .gate("br")) transistor_114 (.in(1'b0), .out(LP8), .gate(transistor_122_out));
  Transistor #(.\type ("n")) transistor_115 (.in(1'b0), .out(transistor_115_out), .gate(F3));
  Transistor #(.\type ("n")) transistor_116 (.in(1'b0), .out(transistor_115_out), .gate(F2));
  Transistor #(.\type ("n")) transistor_117 (.in(1'b0), .out(transistor_115_out), .gate(not_3_out));
  Transistor #(.\type ("n")) transistor_118 (.in(1'b0), .out(transistor_115_out), .gate(F0));
  Pull_Resistor #(.pull(1)) pull_resistor_14 (.node(transistor_115_out));
  Transistor #(.\type ("n"), .gate("br")) transistor_119 (.in(1'b0), .out(LP1), .gate(transistor_123_out));
  Transistor #(.\type ("n"), .gate("br")) transistor_120 (.in(1'b0), .out(LP5), .gate(transistor_123_out));
  Transistor #(.\type ("n"), .gate("br")) transistor_121 (.in(1'b0), .out(LP6), .gate(transistor_123_out));
  Transistor #(.\type ("n")) transistor_122 (.in(1'b0), .out(transistor_122_out), .gate(F3));
  Transistor #(.\type ("n")) transistor_123 (.in(1'b0), .out(transistor_123_out), .gate(F3));
  Transistor #(.\type ("n")) transistor_124 (.in(1'b0), .out(transistor_123_out), .gate(F2));
  Transistor #(.\type ("n")) transistor_125 (.in(1'b0), .out(transistor_122_out), .gate(F2));
  Transistor #(.\type ("n")) transistor_126 (.in(1'b0), .out(transistor_123_out), .gate(F1));
  Transistor #(.\type ("n")) transistor_127 (.in(1'b0), .out(transistor_122_out), .gate(F1));
  Transistor #(.\type ("n")) transistor_128 (.in(1'b0), .out(transistor_123_out), .gate(F0));
  Transistor #(.\type ("n")) transistor_129 (.in(1'b0), .out(transistor_122_out), .gate(not_4_out));
  Pull_Resistor #(.pull(1)) pull_resistor_15 (.node(transistor_123_out));
  Pull_Resistor #(.pull(1)) pull_resistor_16 (.node(transistor_122_out));
  Pull_Resistor #(.pull(1)) pull_resistor_17 (.node(LP0));
  Pull_Resistor #(.pull(1)) pull_resistor_18 (.node(LP1));
  Pull_Resistor #(.pull(1)) pull_resistor_19 (.node(LP2));
  Pull_Resistor #(.pull(1)) pull_resistor_20 (.node(LP3));
  Pull_Resistor #(.pull(1)) pull_resistor_21 (.node(LP4));
  Pull_Resistor #(.pull(1)) pull_resistor_22 (.node(LP5));
  Pull_Resistor #(.pull(1)) pull_resistor_23 (.node(LP6));
  Pull_Resistor #(.pull(1)) pull_resistor_24 (.node(LP7));
  Pull_Resistor #(.pull(1)) pull_resistor_25 (.node(LP8));
endmodule

module DPCM_SAMPLE_BIT_COUNTER (
  input  nACLK,
  input  RES,
  input  NSTEP,
  output NOUT
);

  wire d_ff_1_q, d_ff_1_qn, d_ff_2_q, d_ff_2_qn, d_ff_3_q, d_ff_3_qn, d_ff_4_qn, d_ff_5_qn, d_ff_6_qn,
       multiplexer_1_out, multiplexer_2_out, multiplexer_3_out, nor_1_out, nor_2_out, nor_3_out, not_1_out,
       not_2_out, not_3_out;

  D_Flip_Flop d_ff_1 (.clk(NSTEP), .D(d_ff_4_qn), .Q(d_ff_1_q), .Qn(d_ff_1_qn), .reset(RES));  // open: preset, en
  D_Flip_Flop d_ff_2 (.clk(NSTEP), .D(d_ff_5_qn), .Q(d_ff_2_q), .Qn(d_ff_2_qn), .reset(RES));  // open: preset, en
  D_Flip_Flop d_ff_3 (.clk(NSTEP), .D(d_ff_6_qn), .Q(d_ff_3_q), .Qn(d_ff_3_qn), .reset(RES));  // open: preset, en
  Multiplexer #(.enable("false")) multiplexer_1 (.in0(d_ff_1_qn), .in1(d_ff_1_q), .out(multiplexer_1_out), .sel(1'b1));
  not not_1 (not_1_out, 1'b1);
  Multiplexer #(.enable("false")) multiplexer_2 (
    .in0(d_ff_2_qn), .in1(d_ff_2_q), .out(multiplexer_2_out), .sel(nor_1_out));
  not not_2 (not_2_out, nor_1_out);
  Multiplexer #(.enable("false")) multiplexer_3 (
    .in0(d_ff_3_qn), .in1(d_ff_3_q), .out(multiplexer_3_out), .sel(nor_2_out));
  not not_3 (not_3_out, nor_2_out);
  D_Flip_Flop d_ff_4 (.clk(nACLK), .D(multiplexer_1_out), .Qn(d_ff_4_qn));  // open: Q, preset, en, reset
  D_Flip_Flop d_ff_5 (.clk(nACLK), .D(multiplexer_2_out), .Qn(d_ff_5_qn));  // open: Q, preset, en, reset
  D_Flip_Flop d_ff_6 (.clk(nACLK), .D(multiplexer_3_out), .Qn(d_ff_6_qn));  // open: Q, preset, en, reset
  nor nor_1 (nor_1_out, d_ff_1_qn, not_1_out);
  nor nor_2 (nor_2_out, d_ff_2_qn, not_2_out);
  nor nor_3 (nor_3_out, d_ff_3_qn, not_3_out);
  D_Flip_Flop d_ff_7 (.clk(nACLK), .D(nor_3_out), .Qn(NOUT));  // open: Q, preset, en, reset
endmodule

// DPCM CONTROL
module DPCM_CONTROL (
  input  ACLK,
  input  nACLK,
  input  PHI1,
  input  D4,
  input  W4015,
  input  nR4015,
  input  ENIRQ,
  input  Res,
  input  LOOP,
  input  SOUT,
  input  R_W,
  input  FLOAD,
  input  DOUT,
  input  NOUT,
  output D4_2,
  output nDMCINT,
  output D7,
  output SSTEP,
  output SLOAD,
  output RUNDMC,
  output out_21,
  output Z4,
  output NSTEP,
  output nFLOAD,
  output DSTEP,
  output PCM,
  output BLOAD,
  output BSTEP
);

  wire and_1_out, and_2_out, and_3_out, d_ff_1_qn, d_ff_2_q, d_ff_3_q, d_ff_4_qn, d_ff_5_q, d_ff_5_qn,
       d_ff_6_q, d_ff_7_qn, d_ff_8_q, d_ff_9_q, d_ff_10_qn, d_ff_11_q, d_ff_12_qn, d_ff_13_q, d_ff_15_qn,
       nand_1_out, nor_1_out, nor_3_out, nor_4_out, nor_6_out, nor_9_out, nor_11_out, not_2_out, not_3_out,
       not_4_out, not_5_out, not_6_out, not_7_out, not_9_out, not_10_out, or_1_out, or_2_out, or_3_out,
       or_4_out, or_5_out, or_6_out, s_r_ff_1_q, s_r_ff_2_qn, s_r_ff_3_qn, s_r_ff_4_qn, s_r_ff_5_q,
       s_r_ff_6_q, s_r_ff_6_qn;

  not not_1 (nFLOAD, FLOAD);
  or or_1 (or_1_out, Res, nor_1_out);
  nor nor_1 (nor_1_out, nFLOAD, NOUT, not_3_out);
  D_Flip_Flop d_ff_1 (.clk(nACLK), .D(d_ff_5_q), .Qn(d_ff_1_qn));  // open: Q, preset, en, reset
  not not_2 (not_2_out, PHI1);
  D_Flip_Flop d_ff_2 (.clk(nACLK), .D(DOUT), .Q(d_ff_2_q));  // open: Qn, preset, en, reset
  D_Flip_Flop d_ff_3 (.clk(nACLK), .D(s_r_ff_1_q), .Q(d_ff_3_q));  // open: Qn, preset, en, reset
  S_R_Flip_Flop #(.trigger("high")) s_r_ff_1 (
    .S(or_1_out), .clk(1'b1), .R(BLOAD), .Q(s_r_ff_1_q));  // open: Qn, preset, reset, en
  not not_3 (not_3_out, d_ff_15_qn);
  not not_4 (not_4_out, ACLK);
  and and_1 (and_1_out, ACLK, W4015);
  or or_2 (or_2_out, W4015, Res, ENIRQ);
  D_Flip_Flop d_ff_4 (.clk(not_4_out), .D(d_ff_1_qn), .Qn(d_ff_4_qn));  // open: Q, preset, en, reset
  nand nand_1 (nand_1_out, not_2_out, R_W);
  nor nor_2 (DSTEP, d_ff_2_q, nFLOAD, d_ff_3_q);
  not not_5 (not_5_out, NOUT);
  D_Flip_Flop #(.trigger("high")) d_ff_5 (
    .clk(and_1_out), .D(D4), .Q(d_ff_5_q), .Qn(d_ff_5_qn), .reset(or_3_out));  // open: preset, en
  or or_3 (or_3_out, Res, nor_9_out);
  D_Flip_Flop d_ff_6 (.clk(nACLK), .D(d_ff_4_qn), .Q(d_ff_6_q));  // open: Qn, preset, en, reset
  D_Flip_Flop d_ff_7 (.clk(nACLK), .D(d_ff_4_qn), .Qn(d_ff_7_qn));  // open: Q, preset, en, reset
  or or_4 (or_4_out, Res, nor_4_out);
  or or_5 (or_5_out, BLOAD, Res);
  S_R_Flip_Flop #(.trigger("high")) s_r_ff_2 (
    .S(PCM), .clk(1'b1), .R(or_4_out), .Qn(s_r_ff_2_qn));  // open: Q, preset, reset, en
  nor nor_3 (nor_3_out, ACLK, d_ff_6_q, d_ff_1_qn);
  D_Flip_Flop d_ff_8 (.clk(nACLK), .D(s_r_ff_2_qn), .Q(d_ff_8_q));  // open: Qn, preset, en, reset
  not not_6 (not_6_out, not_4_out);
  nor nor_4 (nor_4_out, d_ff_8_q, not_6_out);
  nor nor_5 (PCM, PHI1, Z4);
  D_Flip_Flop d_ff_9 (.clk(nACLK), .D(SOUT), .Q(d_ff_9_q));  // open: Qn, preset, en, reset
  D_Flip_Flop d_ff_10 (.clk(nACLK), .D(SOUT), .Qn(d_ff_10_qn));  // open: Q, preset, en, reset
  D_Flip_Flop d_ff_11 (.clk(nACLK), .D(SOUT), .Q(d_ff_11_q));  // open: Qn, preset, en, reset
  not not_7 (not_7_out, s_r_ff_6_qn);
  or or_6 (or_6_out, Res, d_ff_7_qn, not_7_out);
  nor nor_6 (nor_6_out, d_ff_7_qn, not_7_out, nand_1_out);
  and and_2 (and_2_out, d_ff_13_q, nACLK);
  S_R_Flip_Flop #(.trigger("high")) s_r_ff_3 (
    .S(or_6_out), .clk(1'b1), .R(nor_6_out), .Qn(s_r_ff_3_qn));  // open: Q, preset, reset, en
  S_R_Flip_Flop #(.trigger("high")) s_r_ff_4 (
    .S(not_4_out), .clk(1'b1), .R(and_2_out), .Qn(s_r_ff_4_qn));  // open: Q, preset, reset, en
  and and_3 (and_3_out, nor_4_out, d_ff_11_q);
  not not_8 (Z4, s_r_ff_4_qn);
  nor nor_7 (out_21, s_r_ff_3_qn, s_r_ff_4_qn);
  S_R_Flip_Flop #(.trigger("high")) s_r_ff_5 (
    .S(or_2_out), .clk(1'b1), .R(nor_9_out), .Q(s_r_ff_5_q));  // open: Qn, preset, reset, en
  not not_9 (not_9_out, nor_4_out);
  D_Flip_Flop d_ff_12 (.clk(not_4_out), .D(s_r_ff_3_qn), .Qn(d_ff_12_qn));  // open: Q, preset, en, reset
  D_Flip_Flop d_ff_13 (.clk(not_4_out), .D(s_r_ff_3_qn), .Q(d_ff_13_q));  // open: Qn, preset, en, reset
  S_R_Flip_Flop #(.trigger("high")) s_r_ff_6 (
    .S(PCM), .clk(1'b1), .R(or_5_out), .Q(s_r_ff_6_q), .Qn(s_r_ff_6_qn));  // open: preset, reset, en
  assign D4_2 = not_10_out ? ~d_ff_5_qn : 1'bz;  // Controlled_Inverter controlled_inverter_1
  nor nor_8 (nDMCINT, ENIRQ, s_r_ff_5_q);
  assign D7 = not_10_out ? ~s_r_ff_5_q : 1'bz;  // Controlled_Inverter controlled_inverter_2
  not not_10 (not_10_out, nR4015);
  nor nor_9 (nor_9_out, LOOP, d_ff_10_qn, not_9_out);
  nor nor_10 (SSTEP, not_9_out, d_ff_9_q, nor_3_out);
  nor nor_11 (nor_11_out, nor_3_out, and_3_out);
  D_Flip_Flop d_ff_14 (.clk(nACLK), .D(d_ff_12_qn), .Qn(RUNDMC));  // open: Q, preset, en, reset
  D_Flip_Flop d_ff_15 (.clk(nACLK), .D(s_r_ff_6_q), .Qn(d_ff_15_qn));  // open: Q, preset, en, reset
  not not_11 (SLOAD, nor_11_out);
  not not_12 (NSTEP, nFLOAD);
  nor nor_12 (BLOAD, nFLOAD, d_ff_15_qn, NOUT);
  nor nor_13 (BSTEP, nFLOAD, not_5_out);

  // Notes on the sheet:
  //   Inv1
  //   DL12
  //   Nor5
  //   DL3
  //   Inv4
  //   Nor8
  //   DL11
  //   RS2
  //   Inv5
  //   DL6
  //   Inv6
  //   DL5
  //   DL4
  //   RS3
  //   Nor3
  //   DL10
  //   Inv7
  //   Nor8
  //   Nor10
  //   DL14
  //   DL1
  //   DL2
  //   Inv3
  //   Nor4
  //   RS6
  //   RS5
  //   RS1
  //   Inv10
  //   z1
  //   z2
  //   z3
  //   Nor6
  //   RS4
  //   Nor2
  //   Nor+and
  //   DL9
  //   DL8
  //   Nor1
  //   Nor11
  //   DL7
  //   DL13
  //   Inv2
  //   Nor9
  //   Nor7
endmodule

// SAMPLE LENGHT COUNTER
module DPCM_SAMPLE_LENGHT_COUNTER (
  input  nACLK,
  input  SLOAD,
  input  SSTEP,
  input  RES,
  input  LSC0,
  input  LSC1,
  input  LSC2,
  input  LSC3,
  input  LSC4,
  input  LSC5,
  input  LSC6,
  input  LSC7,
  output SOUT
);

  wire and_1_out, and_2_out, and_3_out, and_4_out, and_5_out, and_6_out, and_7_out, and_8_out, and_9_out,
       and_10_out, and_11_out, and_12_out, and_13_out, and_14_out, and_15_out, and_16_out, d_ff_1_qn,
       d_ff_2_qn, d_ff_3_qn, d_ff_4_qn, d_ff_5_qn, d_ff_6_qn, d_ff_7_qn, d_ff_8_qn, d_ff_9_qn, d_ff_10_qn,
       d_ff_11_qn, d_ff_12_qn, d_ff_13_qn, d_ff_14_qn, d_ff_15_qn, d_ff_16_qn, d_ff_17_qn, d_ff_18_qn,
       d_ff_19_qn, d_ff_20_qn, d_ff_21_qn, d_ff_22_qn, d_ff_23_qn, d_ff_24_qn, d_ff_25_q, d_ff_25_qn,
       multiplexer_1_out, multiplexer_2_out, multiplexer_3_out, multiplexer_4_out, multiplexer_5_out,
       multiplexer_6_out, multiplexer_7_out, multiplexer_8_out, multiplexer_9_out, multiplexer_10_out,
       multiplexer_11_out, multiplexer_12_out, nor_1_out, nor_2_out, nor_3_out, nor_4_out, nor_5_out,
       nor_6_out, nor_7_out, nor_8_out, nor_9_out, nor_10_out, nor_11_out, not_1_out, not_2_out, not_3_out,
       not_4_out, not_5_out, not_6_out, not_7_out, not_8_out, not_9_out, not_10_out, not_11_out, not_12_out,
       not_13_out, not_14_out, not_15_out, not_16_out, not_17_out, not_18_out, not_19_out, not_20_out,
       not_21_out, or_1_out, or_2_out, or_3_out, or_4_out, or_5_out, or_6_out, or_7_out, or_8_out, or_9_out,
       or_10_out, or_11_out, or_12_out, undriven, undriven_2, undriven_3;
  wire [11:0] counter_1_q, d_ff_1_q;

  not not_1 (not_1_out, LSC0);
  not not_2 (not_2_out, LSC1);
  not not_3 (not_3_out, LSC2);
  not not_4 (not_4_out, LSC3);
  not not_5 (not_5_out, LSC4);
  not not_6 (not_6_out, LSC5);
  not not_7 (not_7_out, LSC6);
  not not_8 (not_8_out, LSC7);
  D_Flip_Flop d_ff_1 (
    .clk(SSTEP), .D(d_ff_13_qn), .Q(d_ff_1_q[0]), .Qn(d_ff_1_qn), .reset(or_1_out));  // open: preset, en
  or or_1 (or_1_out, SLOAD, RES);
  D_Flip_Flop d_ff_2 (
    .clk(SSTEP), .D(d_ff_14_qn), .Q(d_ff_1_q[1]), .Qn(d_ff_2_qn), .reset(or_2_out));  // open: preset, en
  or or_2 (or_2_out, SLOAD, RES);
  D_Flip_Flop d_ff_3 (
    .clk(SSTEP), .D(d_ff_15_qn), .Q(d_ff_1_q[2]), .Qn(d_ff_3_qn), .reset(or_3_out));  // open: preset, en
  or or_3 (or_3_out, SLOAD, RES);
  D_Flip_Flop d_ff_4 (
    .clk(SSTEP), .D(d_ff_16_qn), .Q(d_ff_1_q[3]), .Qn(d_ff_4_qn), .reset(or_4_out));  // open: preset, en
  or or_4 (or_4_out, SLOAD, RES);
  D_Flip_Flop d_ff_5 (
    .clk(SSTEP), .D(d_ff_17_qn), .Q(d_ff_1_q[4]), .Qn(d_ff_5_qn), .preset(and_1_out), .reset(or_5_out));  // open: en
  and and_1 (and_1_out, LSC0, SLOAD);
  or or_5 (or_5_out, and_2_out, RES);
  and and_2 (and_2_out, SLOAD, not_1_out);
  D_Flip_Flop d_ff_6 (
    .clk(SSTEP), .D(d_ff_18_qn), .Q(d_ff_1_q[5]), .Qn(d_ff_6_qn), .preset(and_3_out), .reset(or_6_out));  // open: en
  and and_3 (and_3_out, LSC1, SLOAD);
  or or_6 (or_6_out, and_4_out, RES);
  and and_4 (and_4_out, SLOAD, not_2_out);
  D_Flip_Flop d_ff_7 (
    .clk(SSTEP), .D(d_ff_19_qn), .Q(d_ff_1_q[6]), .Qn(d_ff_7_qn), .preset(and_5_out), .reset(or_7_out));  // open: en
  or or_7 (or_7_out, and_6_out, RES);
  and and_5 (and_5_out, LSC2, SLOAD);
  and and_6 (and_6_out, SLOAD, not_3_out);
  D_Flip_Flop d_ff_8 (
    .clk(SSTEP), .D(d_ff_20_qn), .Q(d_ff_1_q[7]), .Qn(d_ff_8_qn), .preset(and_7_out), .reset(or_8_out));  // open: en
  or or_8 (or_8_out, and_8_out, RES);
  and and_7 (and_7_out, LSC3, SLOAD);
  and and_8 (and_8_out, SLOAD, not_4_out);
  D_Flip_Flop d_ff_9 (
    .clk(SSTEP), .D(d_ff_21_qn), .Q(d_ff_1_q[8]), .Qn(d_ff_9_qn), .preset(and_9_out), .reset(or_9_out));  // open: en
  and and_9 (and_9_out, LSC4, SLOAD);
  or or_9 (or_9_out, and_10_out, RES);
  and and_10 (and_10_out, SLOAD, not_5_out);
  D_Flip_Flop d_ff_10 (
    .clk(SSTEP), .D(d_ff_22_qn), .Q(d_ff_1_q[9]), .Qn(d_ff_10_qn), .preset(and_11_out), .reset(or_10_out));  // open: en
  and and_11 (and_11_out, LSC5, SLOAD);
  or or_10 (or_10_out, and_12_out, RES);
  and and_12 (and_12_out, SLOAD, not_6_out);
  D_Flip_Flop d_ff_11 (
    .clk(SSTEP), .D(d_ff_23_qn), .Q(d_ff_1_q[10]), .Qn(d_ff_11_qn), .preset(and_13_out), .reset(or_11_out));  // open: en
  and and_13 (and_13_out, LSC6, SLOAD);
  or or_11 (or_11_out, and_14_out, RES);
  and and_14 (and_14_out, SLOAD, not_7_out);
  D_Flip_Flop d_ff_12 (
    .clk(SSTEP), .D(d_ff_24_qn), .Q(d_ff_1_q[11]), .Qn(d_ff_12_qn), .preset(and_15_out), .reset(or_12_out));  // open: en
  or or_12 (or_12_out, and_16_out, RES);
  and and_15 (and_15_out, LSC7, SLOAD);
  and and_16 (and_16_out, SLOAD, not_8_out);
  Multiplexer multiplexer_1 (.in0(d_ff_1_qn), .in1(d_ff_1_q[0]), .out(multiplexer_1_out), .sel(1'b1));  // open: en
  not not_9 (not_9_out, 1'b1);
  Multiplexer multiplexer_2 (.in0(d_ff_2_qn), .in1(d_ff_1_q[1]), .out(multiplexer_2_out), .sel(nor_1_out));  // open: en
  not not_10 (not_10_out, nor_1_out);
  Multiplexer multiplexer_3 (.in0(d_ff_3_qn), .in1(d_ff_1_q[2]), .out(multiplexer_3_out), .sel(nor_2_out));  // open: en
  not not_11 (not_11_out, nor_2_out);
  Multiplexer multiplexer_4 (.in0(d_ff_4_qn), .in1(d_ff_1_q[3]), .out(multiplexer_4_out), .sel(nor_3_out));  // open: en
  not not_12 (not_12_out, nor_3_out);
  Multiplexer multiplexer_5 (.in0(d_ff_5_qn), .in1(d_ff_1_q[4]), .out(multiplexer_5_out), .sel(nor_4_out));  // open: en
  not not_13 (not_13_out, nor_4_out);
  Multiplexer multiplexer_6 (.in0(d_ff_6_qn), .in1(d_ff_1_q[5]), .out(multiplexer_6_out), .sel(nor_5_out));  // open: en
  not not_14 (not_14_out, nor_5_out);
  Multiplexer multiplexer_7 (.in0(d_ff_7_qn), .in1(d_ff_1_q[6]), .out(multiplexer_7_out), .sel(nor_6_out));  // open: en
  not not_15 (not_15_out, nor_6_out);
  Multiplexer multiplexer_8 (.in0(d_ff_8_qn), .in1(d_ff_1_q[7]), .out(multiplexer_8_out), .sel(nor_7_out));  // open: en
  not not_16 (not_16_out, nor_7_out);
  Multiplexer multiplexer_9 (.in0(d_ff_9_qn), .in1(d_ff_1_q[8]), .out(multiplexer_9_out), .sel(nor_8_out));  // open: en
  not not_17 (not_17_out, nor_8_out);
  Multiplexer multiplexer_10 (
    .in0(d_ff_10_qn), .in1(d_ff_1_q[9]), .out(multiplexer_10_out), .sel(nor_9_out));  // open: en
  not not_18 (not_18_out, nor_9_out);
  Multiplexer multiplexer_11 (
    .in0(d_ff_11_qn), .in1(d_ff_1_q[10]), .out(multiplexer_11_out), .sel(nor_10_out));  // open: en
  not not_19 (not_19_out, nor_10_out);
  Multiplexer multiplexer_12 (
    .in0(d_ff_12_qn), .in1(d_ff_1_q[11]), .out(multiplexer_12_out), .sel(nor_11_out));  // open: en
  not not_20 (not_20_out, nor_11_out);
  D_Flip_Flop d_ff_13 (.clk(nACLK), .D(multiplexer_1_out), .Qn(d_ff_13_qn));  // open: Q, preset, en, reset
  D_Flip_Flop d_ff_14 (.clk(nACLK), .D(multiplexer_2_out), .Qn(d_ff_14_qn));  // open: Q, preset, en, reset
  D_Flip_Flop d_ff_15 (.clk(nACLK), .D(multiplexer_3_out), .Qn(d_ff_15_qn));  // open: Q, preset, en, reset
  D_Flip_Flop d_ff_16 (.clk(nACLK), .D(multiplexer_4_out), .Qn(d_ff_16_qn));  // open: Q, preset, en, reset
  D_Flip_Flop d_ff_17 (.clk(nACLK), .D(multiplexer_5_out), .Qn(d_ff_17_qn));  // open: Q, preset, en, reset
  D_Flip_Flop d_ff_18 (.clk(nACLK), .D(multiplexer_6_out), .Qn(d_ff_18_qn));  // open: Q, preset, en, reset
  D_Flip_Flop d_ff_19 (.clk(nACLK), .D(multiplexer_7_out), .Qn(d_ff_19_qn));  // open: Q, preset, en, reset
  D_Flip_Flop d_ff_20 (.clk(nACLK), .D(multiplexer_8_out), .Qn(d_ff_20_qn));  // open: Q, preset, en, reset
  D_Flip_Flop d_ff_21 (.clk(nACLK), .D(multiplexer_9_out), .Qn(d_ff_21_qn));  // open: Q, preset, en, reset
  D_Flip_Flop d_ff_22 (.clk(nACLK), .D(multiplexer_10_out), .Qn(d_ff_22_qn));  // open: Q, preset, en, reset
  D_Flip_Flop d_ff_23 (.clk(nACLK), .D(multiplexer_11_out), .Qn(d_ff_23_qn));  // open: Q, preset, en, reset
  D_Flip_Flop d_ff_24 (.clk(nACLK), .D(multiplexer_12_out), .Qn(d_ff_24_qn));  // open: Q, preset, en, reset
  nor nor_1 (nor_1_out, d_ff_1_q[0], not_9_out);
  nor nor_2 (nor_2_out, d_ff_1_q[1], not_10_out);
  nor nor_3 (nor_3_out, d_ff_1_q[2], not_11_out);
  nor nor_4 (nor_4_out, d_ff_1_q[3], not_12_out);
  nor nor_5 (nor_5_out, d_ff_1_q[4], not_13_out);
  nor nor_6 (nor_6_out, d_ff_1_q[5], not_14_out);
  nor nor_7 (nor_7_out, d_ff_1_q[6], not_15_out);
  nor nor_8 (nor_8_out, d_ff_1_q[7], not_16_out);
  nor nor_9 (nor_9_out, d_ff_1_q[8], not_17_out);
  nor nor_10 (nor_10_out, d_ff_1_q[9], not_18_out);
  nor nor_11 (nor_11_out, d_ff_1_q[10], not_19_out);
  nor nor_12 (SOUT, d_ff_1_q[11], not_20_out);
  not not_21 (not_21_out, undriven_2);
  Counter #(.width(12), .max('hfff)) counter_1 (
    .Q(counter_1_q), .clk(undriven), .clr(not_21_out));  // open: load, D, count, carry
  D_Flip_Flop #(.trigger("high")) d_ff_25 (
    .clk(undriven), .D(SOUT), .Q(d_ff_25_q), .Qn(d_ff_25_qn), .reset(undriven_3));  // open: preset, en
  Register #(.width(12), .trigger("high")) register_1 (
    .D(counter_1_q), .clk(d_ff_25_q), .clr(undriven_3));  // open: en, Q
  // Probe on d_ff_1_q
endmodule
// ADDRESS COUNTER
module DPCM_ADDRESS_COUNTER (
  input  nACLK,
  input  SLOAD,
  input  SSTEP,
  input  RES,
  input  LDMC6,
  input  LDMC7,
  input  LDMC8,
  input  LDMC9,
  input  LDMC10,
  input  LDMC11,
  input  LDMC12,
  input  LDMC13,
  output DMC_A0,
  output DMC_A1,
  output DMC_A2,
  output DMC_A3,
  output DMC_A4,
  output DMC_A5,
  output DMC_A6,
  output DMC_A7,
  output DMC_A8,
  output DMC_A9,
  output DMC_A10,
  output DMC_A11,
  output DMC_A12,
  output DMC_A13,
  output DMC_A14
);

  wire and_1_out, and_2_out, and_3_out, and_4_out, and_5_out, and_6_out, and_7_out, and_8_out, and_9_out,
       and_10_out, and_11_out, and_12_out, and_13_out, and_14_out, and_15_out, and_16_out, and_17_out,
       d_ff_1_qn, d_ff_2_qn, d_ff_3_qn, d_ff_4_qn, d_ff_5_qn, d_ff_6_qn, d_ff_7_qn, d_ff_8_qn, d_ff_9_qn,
       d_ff_10_qn, d_ff_11_qn, d_ff_12_qn, d_ff_13_qn, d_ff_14_qn, d_ff_15_qn, d_ff_16_qn, d_ff_17_qn,
       d_ff_18_qn, d_ff_19_qn, d_ff_20_qn, d_ff_21_qn, d_ff_22_qn, d_ff_23_qn, d_ff_24_qn, d_ff_25_qn,
       d_ff_26_qn, d_ff_27_qn, d_ff_28_qn, d_ff_29_qn, d_ff_30_qn, multiplexer_1_out, multiplexer_2_out,
       multiplexer_3_out, multiplexer_4_out, multiplexer_5_out, multiplexer_6_out, multiplexer_7_out,
       multiplexer_8_out, multiplexer_9_out, multiplexer_10_out, multiplexer_11_out, multiplexer_12_out,
       multiplexer_13_out, multiplexer_14_out, multiplexer_15_out, nor_1_out, nor_2_out, nor_3_out,
       nor_4_out, nor_5_out, nor_6_out, nor_7_out, nor_8_out, nor_9_out, nor_10_out, nor_11_out, nor_12_out,
       nor_13_out, nor_14_out, not_1_out, not_2_out, not_3_out, not_4_out, not_5_out, not_6_out, not_7_out,
       not_8_out, not_9_out, not_10_out, not_11_out, not_12_out, not_13_out, not_14_out, not_15_out,
       not_16_out, not_17_out, not_18_out, not_19_out, not_20_out, not_21_out, not_22_out, or_1_out,
       or_2_out, or_3_out, or_4_out, or_5_out, or_6_out, or_7_out, or_8_out, or_9_out, or_10_out, or_11_out,
       or_12_out, or_13_out, or_14_out;

  not not_1 (not_1_out, LDMC6);
  not not_2 (not_2_out, LDMC7);
  not not_3 (not_3_out, LDMC8);
  not not_4 (not_4_out, LDMC9);
  not not_5 (not_5_out, LDMC10);
  not not_6 (not_6_out, LDMC11);
  not not_7 (not_7_out, LDMC12);
  not not_8 (not_8_out, LDMC13);
  or or_1 (or_1_out, SLOAD, RES);
  or or_2 (or_2_out, SLOAD, RES);
  or or_3 (or_3_out, SLOAD, RES);
  or or_4 (or_4_out, SLOAD, RES);
  or or_5 (or_5_out, SLOAD, RES);
  or or_6 (or_6_out, SLOAD, RES);
  or or_7 (or_7_out, and_2_out, RES);
  and and_1 (and_1_out, LDMC6, SLOAD);
  and and_2 (and_2_out, SLOAD, not_1_out);
  and and_3 (and_3_out, LDMC7, SLOAD);
  or or_8 (or_8_out, and_4_out, RES);
  and and_4 (and_4_out, SLOAD, not_2_out);
  and and_5 (and_5_out, LDMC8, SLOAD);
  or or_9 (or_9_out, and_6_out, RES);
  and and_6 (and_6_out, SLOAD, not_3_out);
  and and_7 (and_7_out, LDMC9, SLOAD);
  or or_10 (or_10_out, and_8_out, RES);
  and and_8 (and_8_out, SLOAD, not_4_out);
  and and_9 (and_9_out, LDMC10, SLOAD);
  or or_11 (or_11_out, and_10_out, RES);
  and and_10 (and_10_out, SLOAD, not_5_out);
  and and_11 (and_11_out, LDMC11, SLOAD);
  or or_12 (or_12_out, and_12_out, RES);
  and and_12 (and_12_out, SLOAD, not_6_out);
  or or_13 (or_13_out, and_14_out, RES);
  and and_13 (and_13_out, LDMC12, SLOAD);
  and and_14 (and_14_out, SLOAD, not_7_out);
  and and_15 (and_15_out, LDMC13, SLOAD);
  or or_14 (or_14_out, and_16_out, RES);
  and and_16 (and_16_out, SLOAD, not_8_out);
  and and_17 (and_17_out, SLOAD, 1'b1);
  D_Flip_Flop d_ff_1 (.clk(SSTEP), .D(d_ff_16_qn), .Q(DMC_A0), .Qn(d_ff_1_qn), .reset(or_1_out));  // open: preset, en
  not not_9 (not_9_out, 1'b1);
  D_Flip_Flop d_ff_2 (.clk(SSTEP), .D(d_ff_17_qn), .Q(DMC_A1), .Qn(d_ff_2_qn), .reset(or_2_out));  // open: preset, en
  not not_10 (not_10_out, nor_1_out);
  D_Flip_Flop d_ff_3 (.clk(SSTEP), .D(d_ff_18_qn), .Q(DMC_A2), .Qn(d_ff_3_qn), .reset(or_3_out));  // open: preset, en
  not not_11 (not_11_out, nor_2_out);
  D_Flip_Flop d_ff_4 (.clk(SSTEP), .D(d_ff_19_qn), .Q(DMC_A3), .Qn(d_ff_4_qn), .reset(or_4_out));  // open: preset, en
  not not_12 (not_12_out, nor_3_out);
  D_Flip_Flop d_ff_5 (.clk(SSTEP), .D(d_ff_20_qn), .Q(DMC_A4), .Qn(d_ff_5_qn), .reset(or_5_out));  // open: preset, en
  not not_13 (not_13_out, nor_4_out);
  D_Flip_Flop d_ff_6 (.clk(SSTEP), .D(d_ff_21_qn), .Q(DMC_A5), .Qn(d_ff_6_qn), .reset(or_6_out));  // open: preset, en
  not not_14 (not_14_out, nor_5_out);
  D_Flip_Flop d_ff_7 (
    .clk(SSTEP), .D(d_ff_22_qn), .Q(DMC_A6), .Qn(d_ff_7_qn), .preset(and_1_out), .reset(or_7_out));  // open: en
  not not_15 (not_15_out, nor_6_out);
  D_Flip_Flop d_ff_8 (
    .clk(SSTEP), .D(d_ff_23_qn), .Q(DMC_A7), .Qn(d_ff_8_qn), .preset(and_3_out), .reset(or_8_out));  // open: en
  not not_16 (not_16_out, nor_7_out);
  D_Flip_Flop d_ff_9 (
    .clk(SSTEP), .D(d_ff_24_qn), .Q(DMC_A8), .Qn(d_ff_9_qn), .preset(and_5_out), .reset(or_9_out));  // open: en
  not not_17 (not_17_out, nor_8_out);
  D_Flip_Flop d_ff_10 (
    .clk(SSTEP), .D(d_ff_25_qn), .Q(DMC_A9), .Qn(d_ff_10_qn), .preset(and_7_out), .reset(or_10_out));  // open: en
  not not_18 (not_18_out, nor_9_out);
  D_Flip_Flop d_ff_11 (
    .clk(SSTEP), .D(d_ff_26_qn), .Q(DMC_A10), .Qn(d_ff_11_qn), .preset(and_9_out), .reset(or_11_out));  // open: en
  not not_19 (not_19_out, nor_10_out);
  D_Flip_Flop d_ff_12 (
    .clk(SSTEP), .D(d_ff_27_qn), .Q(DMC_A11), .Qn(d_ff_12_qn), .preset(and_11_out), .reset(or_12_out));  // open: en
  not not_20 (not_20_out, nor_11_out);
  D_Flip_Flop d_ff_13 (
    .clk(SSTEP), .D(d_ff_28_qn), .Q(DMC_A12), .Qn(d_ff_13_qn), .preset(and_13_out), .reset(or_13_out));  // open: en
  not not_21 (not_21_out, nor_12_out);
  D_Flip_Flop d_ff_14 (
    .clk(SSTEP), .D(d_ff_29_qn), .Q(DMC_A13), .Qn(d_ff_14_qn), .preset(and_15_out), .reset(or_14_out));  // open: en
  not not_22 (not_22_out, nor_13_out);
  D_Flip_Flop d_ff_15 (
    .clk(SSTEP), .D(d_ff_30_qn), .Q(DMC_A14), .Qn(d_ff_15_qn), .preset(and_17_out), .reset(RES));  // open: en
  D_Flip_Flop d_ff_16 (.clk(nACLK), .D(multiplexer_1_out), .Qn(d_ff_16_qn));  // open: Q, preset, en, reset
  Multiplexer multiplexer_1 (.in0(d_ff_1_qn), .in1(DMC_A0), .out(multiplexer_1_out), .sel(1'b1));  // open: en
  D_Flip_Flop d_ff_17 (.clk(nACLK), .D(multiplexer_2_out), .Qn(d_ff_17_qn));  // open: Q, preset, en, reset
  Multiplexer multiplexer_2 (.in0(d_ff_2_qn), .in1(DMC_A1), .out(multiplexer_2_out), .sel(nor_1_out));  // open: en
  D_Flip_Flop d_ff_18 (.clk(nACLK), .D(multiplexer_3_out), .Qn(d_ff_18_qn));  // open: Q, preset, en, reset
  Multiplexer multiplexer_3 (.in0(d_ff_3_qn), .in1(DMC_A2), .out(multiplexer_3_out), .sel(nor_2_out));  // open: en
  D_Flip_Flop d_ff_19 (.clk(nACLK), .D(multiplexer_4_out), .Qn(d_ff_19_qn));  // open: Q, preset, en, reset
  Multiplexer multiplexer_4 (.in0(d_ff_4_qn), .in1(DMC_A3), .out(multiplexer_4_out), .sel(nor_3_out));  // open: en
  D_Flip_Flop d_ff_20 (.clk(nACLK), .D(multiplexer_5_out), .Qn(d_ff_20_qn));  // open: Q, preset, en, reset
  Multiplexer multiplexer_5 (.in0(d_ff_5_qn), .in1(DMC_A4), .out(multiplexer_5_out), .sel(nor_4_out));  // open: en
  D_Flip_Flop d_ff_21 (.clk(nACLK), .D(multiplexer_6_out), .Qn(d_ff_21_qn));  // open: Q, preset, en, reset
  Multiplexer multiplexer_6 (.in0(d_ff_6_qn), .in1(DMC_A5), .out(multiplexer_6_out), .sel(nor_5_out));  // open: en
  D_Flip_Flop d_ff_22 (.clk(nACLK), .D(multiplexer_7_out), .Qn(d_ff_22_qn));  // open: Q, preset, en, reset
  Multiplexer multiplexer_7 (.in0(d_ff_7_qn), .in1(DMC_A6), .out(multiplexer_7_out), .sel(nor_6_out));  // open: en
  D_Flip_Flop d_ff_23 (.clk(nACLK), .D(multiplexer_8_out), .Qn(d_ff_23_qn));  // open: Q, preset, en, reset
  Multiplexer multiplexer_8 (.in0(d_ff_8_qn), .in1(DMC_A7), .out(multiplexer_8_out), .sel(nor_7_out));  // open: en
  D_Flip_Flop d_ff_24 (.clk(nACLK), .D(multiplexer_9_out), .Qn(d_ff_24_qn));  // open: Q, preset, en, reset
  Multiplexer multiplexer_9 (.in0(d_ff_9_qn), .in1(DMC_A8), .out(multiplexer_9_out), .sel(nor_8_out));  // open: en
  D_Flip_Flop d_ff_25 (.clk(nACLK), .D(multiplexer_10_out), .Qn(d_ff_25_qn));  // open: Q, preset, en, reset
  Multiplexer multiplexer_10 (.in0(d_ff_10_qn), .in1(DMC_A9), .out(multiplexer_10_out), .sel(nor_9_out));  // open: en
  D_Flip_Flop d_ff_26 (.clk(nACLK), .D(multiplexer_11_out), .Qn(d_ff_26_qn));  // open: Q, preset, en, reset
  Multiplexer multiplexer_11 (.in0(d_ff_11_qn), .in1(DMC_A10), .out(multiplexer_11_out), .sel(nor_10_out));  // open: en
  D_Flip_Flop d_ff_27 (.clk(nACLK), .D(multiplexer_12_out), .Qn(d_ff_27_qn));  // open: Q, preset, en, reset
  Multiplexer multiplexer_12 (.in0(d_ff_12_qn), .in1(DMC_A11), .out(multiplexer_12_out), .sel(nor_11_out));  // open: en
  D_Flip_Flop d_ff_28 (.clk(nACLK), .D(multiplexer_13_out), .Qn(d_ff_28_qn));  // open: Q, preset, en, reset
  Multiplexer multiplexer_13 (.in0(d_ff_13_qn), .in1(DMC_A12), .out(multiplexer_13_out), .sel(nor_12_out));  // open: en
  D_Flip_Flop d_ff_29 (.clk(nACLK), .D(multiplexer_14_out), .Qn(d_ff_29_qn));  // open: Q, preset, en, reset
  Multiplexer multiplexer_14 (.in0(d_ff_14_qn), .in1(DMC_A13), .out(multiplexer_14_out), .sel(nor_13_out));  // open: en
  D_Flip_Flop d_ff_30 (.clk(nACLK), .D(multiplexer_15_out), .Qn(d_ff_30_qn));  // open: Q, preset, en, reset
  Multiplexer multiplexer_15 (.in0(d_ff_15_qn), .in1(DMC_A14), .out(multiplexer_15_out), .sel(nor_14_out));  // open: en
  nor nor_1 (nor_1_out, d_ff_1_qn, not_9_out);
  nor nor_2 (nor_2_out, d_ff_2_qn, not_10_out);
  nor nor_3 (nor_3_out, d_ff_3_qn, not_11_out);
  nor nor_4 (nor_4_out, d_ff_4_qn, not_12_out);
  nor nor_5 (nor_5_out, d_ff_5_qn, not_13_out);
  nor nor_6 (nor_6_out, d_ff_6_qn, not_14_out);
  nor nor_7 (nor_7_out, d_ff_7_qn, not_15_out);
  nor nor_8 (nor_8_out, d_ff_8_qn, not_16_out);
  nor nor_9 (nor_9_out, d_ff_9_qn, not_17_out);
  nor nor_10 (nor_10_out, d_ff_10_qn, not_18_out);
  nor nor_11 (nor_11_out, d_ff_11_qn, not_19_out);
  nor nor_12 (nor_12_out, d_ff_12_qn, not_20_out);
  nor nor_13 (nor_13_out, d_ff_13_qn, not_21_out);
  nor nor_14 (nor_14_out, d_ff_14_qn, not_22_out);
  // Probe on {1'b1, DMC_A14, DMC_A13, DMC_A12, DMC_A11, DMC_A10, DMC_A9, DMC_A8, DMC_A7, DMC_A6, DMC_A5, DMC_A4, DMC_A3, DMC_A2, DMC_A1, DMC_A0}
endmodule

// OUTPUT COUNTER
module DPCM_OUTPUT_COUNTER (
  input  nACLK,
  input  ACLK,
  input  W4011,
  input  DSTEP,
  input  RES,
  input  BOUT,
  input  DL0,
  input  DL1,
  input  DL2,
  input  DL3,
  input  DL4,
  input  DL5,
  input  DL6,
  output DMC0,
  output DMC1,
  output DMC2,
  output DMC3,
  output DMC4,
  output DMC5,
  output DMC6,
  output DOUT
);

  wire and_1_out, and_2_out, and_3_out, and_4_out, and_5_out, and_6_out, and_7_out, and_8_out, and_9_out,
       and_10_out, and_11_out, and_12_out, and_13_out, and_14_out, d_ff_2_qn, d_ff_3_qn, d_ff_4_qn,
       d_ff_5_qn, d_ff_6_qn, d_ff_7_qn, d_ff_8_q, d_ff_9_q, d_ff_10_q, d_ff_11_q, d_ff_12_q, d_ff_13_q,
       multiplexer_1_out, multiplexer_2_out, multiplexer_3_out, multiplexer_4_out, multiplexer_5_out,
       multiplexer_6_out, multiplexer_7_out, multiplexer_8_out, multiplexer_9_out, multiplexer_10_out,
       multiplexer_11_out, multiplexer_12_out, nor_1_out, nor_2_out, nor_3_out, nor_4_out, nor_5_out,
       not_1_out, not_2_out, not_3_out, not_4_out, not_5_out, not_6_out, not_7_out, not_8_out, not_9_out,
       not_10_out, not_11_out, not_12_out, or_1_out, or_2_out, or_3_out, or_4_out, or_5_out, or_6_out;

  and and_1 (and_1_out, ACLK, W4011);
  not not_1 (not_1_out, DL1);
  not not_2 (not_2_out, DL2);
  not not_3 (not_3_out, DL3);
  not not_4 (not_4_out, DL4);
  not not_5 (not_5_out, DL5);
  not not_6 (not_6_out, DL6);
  and and_2 (and_2_out, W4011, ACLK);
  and and_3 (and_3_out, DL1, and_1_out);
  and and_4 (and_4_out, not_1_out, and_1_out);
  and and_5 (and_5_out, DL2, and_1_out);
  and and_6 (and_6_out, not_2_out, and_1_out);
  and and_7 (and_7_out, DL3, and_1_out);
  and and_8 (and_8_out, not_3_out, and_1_out);
  and and_9 (and_9_out, DL4, and_1_out);
  and and_10 (and_10_out, not_4_out, and_1_out);
  and and_11 (and_11_out, DL5, and_1_out);
  and and_12 (and_12_out, not_5_out, and_1_out);
  and and_13 (and_13_out, DL6, and_1_out);
  and and_14 (and_14_out, not_6_out, and_1_out);
  D_Flip_Flop #(.trigger("high")) d_ff_1 (.clk(and_2_out), .D(DL0), .Q(DMC0));  // open: Qn, preset, en, reset
  D_Flip_Flop d_ff_2 (
    .clk(DSTEP), .D(d_ff_8_q), .Q(DMC1), .Qn(d_ff_2_qn), .preset(and_3_out), .reset(or_1_out));  // open: en
  or or_1 (or_1_out, RES, and_4_out);
  D_Flip_Flop d_ff_3 (
    .clk(DSTEP), .D(d_ff_9_q), .Q(DMC2), .Qn(d_ff_3_qn), .preset(and_5_out), .reset(or_2_out));  // open: en
  or or_2 (or_2_out, RES, and_6_out);
  D_Flip_Flop d_ff_4 (
    .clk(DSTEP), .D(d_ff_10_q), .Q(DMC3), .Qn(d_ff_4_qn), .preset(and_7_out), .reset(or_3_out));  // open: en
  or or_3 (or_3_out, RES, and_8_out);
  D_Flip_Flop d_ff_5 (
    .clk(DSTEP), .D(d_ff_11_q), .Q(DMC4), .Qn(d_ff_5_qn), .preset(and_9_out), .reset(or_4_out));  // open: en
  or or_4 (or_4_out, RES, and_10_out);
  D_Flip_Flop d_ff_6 (
    .clk(DSTEP), .D(d_ff_12_q), .Q(DMC5), .Qn(d_ff_6_qn), .preset(and_11_out), .reset(or_5_out));  // open: en
  or or_5 (or_5_out, RES, and_12_out);
  D_Flip_Flop d_ff_7 (
    .clk(DSTEP), .D(d_ff_13_q), .Q(DMC6), .Qn(d_ff_7_qn), .preset(and_13_out), .reset(or_6_out));  // open: en
  or or_6 (or_6_out, RES, and_14_out);
  Multiplexer multiplexer_1 (.in0(DMC1), .in1(d_ff_2_qn), .out(multiplexer_1_out), .sel(1'b1));  // open: en
  not not_7 (not_7_out, 1'b1);
  Multiplexer multiplexer_2 (.in0(DMC2), .in1(d_ff_3_qn), .out(multiplexer_2_out), .sel(nor_1_out));  // open: en
  not not_8 (not_8_out, nor_1_out);
  Multiplexer multiplexer_3 (.in0(DMC3), .in1(d_ff_4_qn), .out(multiplexer_3_out), .sel(nor_2_out));  // open: en
  not not_9 (not_9_out, nor_2_out);
  Multiplexer multiplexer_4 (.in0(DMC4), .in1(d_ff_5_qn), .out(multiplexer_4_out), .sel(nor_3_out));  // open: en
  not not_10 (not_10_out, nor_3_out);
  Multiplexer multiplexer_5 (.in0(DMC5), .in1(d_ff_6_qn), .out(multiplexer_5_out), .sel(nor_4_out));  // open: en
  not not_11 (not_11_out, nor_4_out);
  Multiplexer multiplexer_6 (.in0(DMC6), .in1(d_ff_7_qn), .out(multiplexer_6_out), .sel(nor_5_out));  // open: en
  not not_12 (not_12_out, nor_5_out);
  Multiplexer multiplexer_7 (.in0(d_ff_2_qn), .in1(DMC1), .out(multiplexer_7_out), .sel(BOUT));  // open: en
  Multiplexer multiplexer_8 (.in0(d_ff_3_qn), .in1(DMC2), .out(multiplexer_8_out), .sel(BOUT));  // open: en
  Multiplexer multiplexer_9 (.in0(d_ff_4_qn), .in1(DMC3), .out(multiplexer_9_out), .sel(BOUT));  // open: en
  Multiplexer multiplexer_10 (.in0(d_ff_5_qn), .in1(DMC4), .out(multiplexer_10_out), .sel(BOUT));  // open: en
  Multiplexer multiplexer_11 (.in0(d_ff_6_qn), .in1(DMC5), .out(multiplexer_11_out), .sel(BOUT));  // open: en
  Multiplexer multiplexer_12 (.in0(d_ff_7_qn), .in1(DMC6), .out(multiplexer_12_out), .sel(BOUT));  // open: en
  nor nor_1 (nor_1_out, multiplexer_7_out, not_7_out);
  nor nor_2 (nor_2_out, multiplexer_8_out, not_8_out);
  nor nor_3 (nor_3_out, multiplexer_9_out, not_9_out);
  nor nor_4 (nor_4_out, multiplexer_10_out, not_10_out);
  nor nor_5 (nor_5_out, multiplexer_11_out, not_11_out);
  nor nor_6 (DOUT, multiplexer_12_out, not_12_out);
  D_Flip_Flop d_ff_8 (.clk(nACLK), .D(multiplexer_1_out), .Q(d_ff_8_q));  // open: Qn, preset, en, reset
  D_Flip_Flop d_ff_9 (.clk(nACLK), .D(multiplexer_2_out), .Q(d_ff_9_q));  // open: Qn, preset, en, reset
  D_Flip_Flop d_ff_10 (.clk(nACLK), .D(multiplexer_3_out), .Q(d_ff_10_q));  // open: Qn, preset, en, reset
  D_Flip_Flop d_ff_11 (.clk(nACLK), .D(multiplexer_4_out), .Q(d_ff_11_q));  // open: Qn, preset, en, reset
  D_Flip_Flop d_ff_12 (.clk(nACLK), .D(multiplexer_5_out), .Q(d_ff_12_q));  // open: Qn, preset, en, reset
  D_Flip_Flop d_ff_13 (.clk(nACLK), .D(multiplexer_6_out), .Q(d_ff_13_q));  // open: Qn, preset, en, reset
  // Probe on {DMC6, DMC5, DMC4, DMC3, DMC2, DMC1}
endmodule

module DPCM_SAMPLE_SHIFT_REGISTER (
  input  ACLK,
  input  nACLK,
  input  SL0,
  input  SL1,
  input  SL2,
  input  SL3,
  input  SL4,
  input  SL5,
  input  SL6,
  input  SL7,
  input  BSTEP,
  input  BLOAD,
  input  res,
  input  PCM,
  output BOUT
);

  wire and_1_out, and_2_out, and_3_out, and_4_out, and_5_out, and_6_out, and_7_out, and_8_out, and_9_out,
       and_10_out, and_11_out, and_12_out, and_13_out, and_14_out, and_15_out, and_16_out, d_ff_1_qn,
       d_ff_2_qn, d_ff_3_qn, d_ff_4_qn, d_ff_5_qn, d_ff_6_qn, d_ff_7_qn, d_ff_8_qn, d_ff_10_q, d_ff_11_q,
       d_ff_12_q, d_ff_13_q, d_ff_14_q, d_ff_15_q, d_ff_16_q, d_ff_17_q, d_ff_18_q, d_ff_19_q, d_ff_20_q,
       d_ff_21_q, d_ff_22_q, d_ff_23_q, not_1_out, not_2_out, not_3_out, not_4_out, not_5_out, not_6_out,
       not_7_out, not_8_out, or_1_out, or_2_out, or_3_out, or_4_out, or_5_out, or_6_out, or_7_out, or_8_out;

  D_Flip_Flop d_ff_1 (.clk(PCM), .D(SL0), .Qn(d_ff_1_qn));  // open: Q, preset, en, reset
  D_Flip_Flop d_ff_2 (.clk(PCM), .D(SL1), .Qn(d_ff_2_qn));  // open: Q, preset, en, reset
  D_Flip_Flop d_ff_3 (.clk(PCM), .D(SL2), .Qn(d_ff_3_qn));  // open: Q, preset, en, reset
  D_Flip_Flop d_ff_4 (.clk(PCM), .D(SL3), .Qn(d_ff_4_qn));  // open: Q, preset, en, reset
  D_Flip_Flop d_ff_5 (.clk(PCM), .D(SL4), .Qn(d_ff_5_qn));  // open: Q, preset, en, reset
  D_Flip_Flop d_ff_6 (.clk(PCM), .D(SL5), .Qn(d_ff_6_qn));  // open: Q, preset, en, reset
  D_Flip_Flop d_ff_7 (.clk(PCM), .D(SL6), .Qn(d_ff_7_qn));  // open: Q, preset, en, reset
  D_Flip_Flop d_ff_8 (.clk(PCM), .D(SL7), .Qn(d_ff_8_qn));  // open: Q, preset, en, reset
  not not_1 (not_1_out, d_ff_1_qn);
  not not_2 (not_2_out, d_ff_2_qn);
  not not_3 (not_3_out, d_ff_3_qn);
  not not_4 (not_4_out, d_ff_4_qn);
  not not_5 (not_5_out, d_ff_5_qn);
  not not_6 (not_6_out, d_ff_6_qn);
  not not_7 (not_7_out, d_ff_7_qn);
  not not_8 (not_8_out, d_ff_8_qn);
  and and_1 (and_1_out, BLOAD, d_ff_1_qn);
  and and_2 (and_2_out, BLOAD, not_1_out);
  and and_3 (and_3_out, BLOAD, d_ff_2_qn);
  and and_4 (and_4_out, BLOAD, not_2_out);
  and and_5 (and_5_out, BLOAD, d_ff_3_qn);
  and and_6 (and_6_out, BLOAD, not_3_out);
  and and_7 (and_7_out, BLOAD, d_ff_4_qn);
  and and_8 (and_8_out, BLOAD, not_4_out);
  and and_9 (and_9_out, BLOAD, d_ff_5_qn);
  and and_10 (and_10_out, BLOAD, not_5_out);
  and and_11 (and_11_out, BLOAD, d_ff_6_qn);
  and and_12 (and_12_out, BLOAD, not_6_out);
  and and_13 (and_13_out, BLOAD, d_ff_7_qn);
  and and_14 (and_14_out, BLOAD, not_7_out);
  and and_15 (and_15_out, BLOAD, d_ff_8_qn);
  and and_16 (and_16_out, BLOAD, not_8_out);
  D_Flip_Flop d_ff_9 (.clk(BSTEP), .D(d_ff_17_q), .Q(BOUT), .preset(or_1_out), .reset(and_2_out));  // open: Qn, en
  or or_1 (or_1_out, and_1_out, res);
  D_Flip_Flop d_ff_10 (
    .clk(BSTEP), .D(d_ff_18_q), .Q(d_ff_10_q), .preset(or_2_out), .reset(and_4_out));  // open: Qn, en
  or or_2 (or_2_out, and_3_out, res);
  D_Flip_Flop d_ff_11 (
    .clk(BSTEP), .D(d_ff_19_q), .Q(d_ff_11_q), .preset(or_3_out), .reset(and_6_out));  // open: Qn, en
  or or_3 (or_3_out, and_5_out, res);
  D_Flip_Flop d_ff_12 (
    .clk(BSTEP), .D(d_ff_20_q), .Q(d_ff_12_q), .preset(or_4_out), .reset(and_8_out));  // open: Qn, en
  or or_4 (or_4_out, and_7_out, res);
  D_Flip_Flop d_ff_13 (
    .clk(BSTEP), .D(d_ff_21_q), .Q(d_ff_13_q), .preset(or_5_out), .reset(and_10_out));  // open: Qn, en
  or or_5 (or_5_out, and_9_out, res);
  D_Flip_Flop d_ff_14 (
    .clk(BSTEP), .D(d_ff_22_q), .Q(d_ff_14_q), .preset(or_6_out), .reset(and_12_out));  // open: Qn, en
  or or_6 (or_6_out, and_11_out, res);
  D_Flip_Flop d_ff_15 (
    .clk(BSTEP), .D(d_ff_23_q), .Q(d_ff_15_q), .preset(or_7_out), .reset(and_14_out));  // open: Qn, en
  or or_7 (or_7_out, and_13_out, res);
  D_Flip_Flop d_ff_16 (.D(1'b0), .Q(d_ff_16_q), .preset(or_8_out), .en(1'b0), .reset(and_16_out));  // open: clk, Qn
  or or_8 (or_8_out, and_15_out, res);
  D_Flip_Flop d_ff_17 (.clk(nACLK), .D(d_ff_10_q), .Q(d_ff_17_q));  // open: Qn, preset, en, reset
  D_Flip_Flop d_ff_18 (.clk(nACLK), .D(d_ff_11_q), .Q(d_ff_18_q));  // open: Qn, preset, en, reset
  D_Flip_Flop d_ff_19 (.clk(nACLK), .D(d_ff_12_q), .Q(d_ff_19_q));  // open: Qn, preset, en, reset
  D_Flip_Flop d_ff_20 (.clk(nACLK), .D(d_ff_13_q), .Q(d_ff_20_q));  // open: Qn, preset, en, reset
  D_Flip_Flop d_ff_21 (.clk(nACLK), .D(d_ff_14_q), .Q(d_ff_21_q));  // open: Qn, preset, en, reset
  D_Flip_Flop d_ff_22 (.clk(nACLK), .D(d_ff_15_q), .Q(d_ff_22_q));  // open: Qn, preset, en, reset
  D_Flip_Flop d_ff_23 (.clk(nACLK), .D(d_ff_16_q), .Q(d_ff_23_q));  // open: Qn, preset, en, reset

  // Notes on the sheet:
  //   SL7 shift register bit connect clock to PHI2 data and enable to ground
  //   Buffer register connect clock to PHI1, enable to PCM
  //   Connect shift registers clock to PHI2, en signal to BSTEP, use latches connected between chains (clock /ACLK)
endmodule

// SPRITE DMA
module SPRITE_DMA (
  input  PHI1,
  input  PHI2,
  input  ACLK,
  input  nACLK,
  input  nR4015,
  input  W4014,
  input  D0,
  input  D1,
  input  D2,
  input  D3,
  input  D4,
  input  D5,
  input  D6,
  input  D7,
  input  RUNDMC,
  input  in_16,
  input  Z4,
  input  R_W,
  input  RES,
  input  CPUA0,
  input  CPUA1,
  input  CPUA2,
  input  CPUA3,
  input  CPUA4,
  input  CPUA5,
  input  CPUA6,
  input  CPUA7,
  input  CPUA8,
  input  CPUA9,
  input  CPUA10,
  input  CPUA11,
  input  CPUA12,
  input  CPUA13,
  input  CPUA14,
  input  CPUA15,
  input  DMC0,
  input  DMC1,
  input  DMC2,
  input  DMC3,
  input  DMC4,
  input  DMC5,
  input  DMC6,
  input  DMC7,
  input  DMC8,
  input  DMC9,
  input  DMC10,
  input  DMC11,
  input  DMC12,
  input  DMC13,
  input  DMC14,
  output R_W__to_R_W_ic_pin,
  output RD,
  output SPRA0,
  output SPRA1,
  output WR,
  output SPRA2,
  output SPRA3,
  output SPRA4,
  output Main_buffer_disable__datapads__disable_1,
  output SPRA5,
  output SPRA6,
  output SPRA7,
  output SPRA8,
  output SPRA9,
  output SPRA10,
  output SPRA11,
  output SPRA12,
  output SPRA13,
  output SPRA14,
  output SPRA15,
  output RDY,
  output CPU_AB,
  output DMC_AB,
  output A0,
  output A1,
  output A2,
  output A3,
  output A4,
  output A5,
  output A6,
  output A7,
  output A8,
  output A9,
  output A10,
  output A11,
  output A12,
  output A13,
  output A14,
  output A15
);

  wire dma_address_counter_1_spre, dma_control_1_spr_cpu, dma_control_1_spr_ppu, dma_control_1_sprs,
       not_1_out;
  wire [7:0] dma_buffer_1_d0o, undriven;

  DMA_ADDRESS_COUNTER dma_address_counter_1 (
    .nACLK(nACLK), .ACLK(ACLK), .SPRS(W4014), .W4014(D0), .RES(D1), .D0(D2), .D1(D3), .D2(D4), .D3(D5),
    .D4(D6), .D5(D7), .D6(RES), .D7(dma_control_1_sprs), .SPR_CPU(dma_control_1_spr_cpu),
    .SPR_PPU(dma_control_1_spr_ppu), .SPRA0(SPRA0), .SPRA1(SPRA1), .SPRA2(SPRA2), .SPRA3(SPRA3),
    .SPRA4(SPRA4), .SPRA5(SPRA5), .SPRA6(SPRA6), .SPRA7(SPRA7), .SPRA8(SPRA8), .SPRA9(SPRA9),
    .SPRA10(SPRA10), .SPRA11(SPRA11), .SPRA12(SPRA12), .SPRA13(SPRA13), .SPRA14(SPRA14), .SPRA15(SPRA15),
    .SPRE(dma_address_counter_1_spre));
  DMA_CONTROL dma_control_1 (
    .ACLK(ACLK), .PHI1(PHI1), .nACLK(nACLK), .W4014(W4014), .SPRE(dma_address_counter_1_spre),
    .RUNDMC(RUNDMC), .in_7(in_16), .R_W(R_W), .RES(RES), .SPRS(dma_control_1_sprs), .RDY(RDY),
    .SPR_PPU(dma_control_1_spr_ppu), .SPR_CPU(dma_control_1_spr_cpu));
  DMA_ADDRESS_MUX dma_address_mux_1 (
    .SPR_PPU(dma_control_1_spr_ppu), .SPR_CPU(dma_control_1_spr_cpu), .Z4(Z4), .SPRA0(SPRA0), .CPUA0(CPUA0),
    .DMC0(DMC0), .SPRA1(SPRA1), .CPUA1(CPUA1), .DMC1(DMC1), .SPRA2(SPRA2), .CPUA2(CPUA2), .DMC2(DMC2),
    .SPRA3(SPRA3), .CPUA3(CPUA3), .DMC3(DMC3), .SPRA4(SPRA4), .CPUA4(CPUA4), .DMC4(DMC4), .SPRA5(SPRA5),
    .CPUA5(CPUA5), .DMC5(DMC5), .SPRA6(SPRA6), .CPUA6(CPUA6), .DMC6(DMC6), .SPRA7(SPRA7), .CPUA7(CPUA7),
    .DMC7(DMC7), .SPRA8(SPRA8), .CPUA8(CPUA8), .DMC8(DMC8), .SPRA9(SPRA9), .CPUA9(CPUA9), .DMC9(DMC9),
    .SPRA10(SPRA10), .CPUA10(CPUA10), .DMC10(DMC10), .SPRA11(SPRA11), .CPUA11(CPUA11), .DMC11(DMC11),
    .SPRA12(SPRA12), .CPUA12(CPUA12), .DMC12(DMC12), .SPRA13(SPRA13), .CPUA13(CPUA13), .DMC13(DMC13),
    .SPRA14(SPRA14), .CPUA14(CPUA14), .DMC14(DMC14), .SPRA15(SPRA15), .CPUA15(CPUA15), .CPU_AB(CPU_AB),
    .DMC_AB(DMC_AB), .A0(A0), .A1(A1), .A2(A2), .A3(A3), .A4(A4), .A5(A5), .A6(A6), .A7(A7), .A8(A8),
    .A9(A9), .A10(A10), .A11(A11), .A12(A12), .A13(A13), .A14(A14), .A15(A15));
  DMA_BUFFER dma_buffer_1 (
    .nR4015(dma_control_1_spr_cpu), .R_W(nR4015), .PHI2(R_W), .SPR_CPU(PHI2),
    .SPR_PPU(dma_control_1_spr_ppu), .WR(WR), ._2R_W(R_W__to_R_W_ic_pin), .D0I(undriven[0]),
    .D0O(dma_buffer_1_d0o[0]), .D1I(undriven[1]), .D1O(dma_buffer_1_d0o[1]), .D2I(undriven[2]),
    .D2O(dma_buffer_1_d0o[2]), .D3I(undriven[3]), .D3O(dma_buffer_1_d0o[3]), .D4I(undriven[4]),
    .D4O(dma_buffer_1_d0o[4]), .D5I(undriven[5]), .D5O(dma_buffer_1_d0o[5]), .D6I(undriven[6]),
    .D6O(dma_buffer_1_d0o[6]), .D7I(undriven[7]), .D7O(dma_buffer_1_d0o[7]));
  not not_1 (not_1_out, R_W__to_R_W_ic_pin);
  not not_2 (RD, not_1_out);
  and and_1 (Main_buffer_disable__datapads__disable_1, RD, WR);

  // Notes on the sheet:
  //   If /R4015 (read 4015) then disable data buffer (2a03 databus become Z)
  //   Databus control
endmodule

// DMA ADDRESS COUNTER
module DMA_ADDRESS_COUNTER (
  input  nACLK,
  input  ACLK,
  input  SPRS,
  input  W4014,
  input  RES,
  input  D0,
  input  D1,
  input  D2,
  input  D3,
  input  D4,
  input  D5,
  input  D6,
  input  D7,
  input  SPR_CPU,
  input  SPR_PPU,
  output SPRA0,
  output SPRA1,
  output SPRA2,
  output SPRA3,
  output SPRA4,
  output SPRA5,
  output SPRA6,
  output SPRA7,
  output SPRA8,
  output SPRA9,
  output SPRA10,
  output SPRA11,
  output SPRA12,
  output SPRA13,
  output SPRA14,
  output SPRA15,
  output SPRE
);

  wire and_1_out, d_ff_1_q, d_ff_1_qn, d_ff_2_q, d_ff_2_qn, d_ff_3_q, d_ff_3_qn, d_ff_4_q, d_ff_4_qn,
       d_ff_5_q, d_ff_5_qn, d_ff_6_q, d_ff_6_qn, d_ff_7_q, d_ff_7_qn, d_ff_8_q, d_ff_8_qn, d_ff_9_q,
       d_ff_10_q, d_ff_11_q, d_ff_12_q, d_ff_13_q, d_ff_14_q, d_ff_15_q, d_ff_16_q, d_ff_17_qn, d_ff_18_qn,
       d_ff_19_qn, d_ff_20_qn, d_ff_21_qn, d_ff_22_qn, d_ff_23_qn, d_ff_24_qn, multiplexer_1_out,
       multiplexer_2_out, multiplexer_3_out, multiplexer_4_out, multiplexer_5_out, multiplexer_6_out,
       multiplexer_7_out, multiplexer_8_out, nor_1_out, nor_2_out, nor_3_out, nor_4_out, nor_5_out,
       nor_6_out, nor_7_out, not_1_out, not_2_out, not_3_out, not_4_out, not_5_out, not_6_out, not_7_out,
       not_8_out, or_1_out, or_2_out, or_3_out, or_4_out, or_5_out, or_6_out, or_7_out, or_8_out;

  or or_1 (or_1_out, W4014, RES);
  or or_2 (or_2_out, W4014, RES);
  or or_3 (or_3_out, W4014, RES);
  or or_4 (or_4_out, W4014, RES);
  or or_5 (or_5_out, W4014, RES);
  or or_6 (or_6_out, W4014, RES);
  or or_7 (or_7_out, W4014, RES);
  or or_8 (or_8_out, W4014, RES);
  and and_1 (and_1_out, W4014, ACLK);
  D_Flip_Flop d_ff_1 (.clk(SPRS), .D(d_ff_17_qn), .Q(d_ff_1_q), .Qn(d_ff_1_qn), .reset(or_1_out));  // open: preset, en
  D_Flip_Flop d_ff_2 (.clk(SPRS), .D(d_ff_18_qn), .Q(d_ff_2_q), .Qn(d_ff_2_qn), .reset(or_2_out));  // open: preset, en
  D_Flip_Flop d_ff_3 (.clk(SPRS), .D(d_ff_19_qn), .Q(d_ff_3_q), .Qn(d_ff_3_qn), .reset(or_3_out));  // open: preset, en
  D_Flip_Flop d_ff_4 (.clk(SPRS), .D(d_ff_20_qn), .Q(d_ff_4_q), .Qn(d_ff_4_qn), .reset(or_4_out));  // open: preset, en
  D_Flip_Flop d_ff_5 (.clk(SPRS), .D(d_ff_21_qn), .Q(d_ff_5_q), .Qn(d_ff_5_qn), .reset(or_5_out));  // open: preset, en
  D_Flip_Flop d_ff_6 (.clk(SPRS), .D(d_ff_22_qn), .Q(d_ff_6_q), .Qn(d_ff_6_qn), .reset(or_6_out));  // open: preset, en
  D_Flip_Flop d_ff_7 (.clk(SPRS), .D(d_ff_23_qn), .Q(d_ff_7_q), .Qn(d_ff_7_qn), .reset(or_7_out));  // open: preset, en
  D_Flip_Flop d_ff_8 (.clk(SPRS), .D(d_ff_24_qn), .Q(d_ff_8_q), .Qn(d_ff_8_qn), .reset(or_8_out));  // open: preset, en
  D_Flip_Flop #(.trigger("high")) d_ff_9 (.clk(and_1_out), .D(D0), .Q(d_ff_9_q));  // open: Qn, preset, en, reset
  D_Flip_Flop #(.trigger("high")) d_ff_10 (.clk(and_1_out), .D(D1), .Q(d_ff_10_q));  // open: Qn, preset, en, reset
  D_Flip_Flop #(.trigger("high")) d_ff_11 (.clk(and_1_out), .D(D2), .Q(d_ff_11_q));  // open: Qn, preset, en, reset
  D_Flip_Flop #(.trigger("high")) d_ff_12 (.clk(and_1_out), .D(D3), .Q(d_ff_12_q));  // open: Qn, preset, en, reset
  D_Flip_Flop #(.trigger("high")) d_ff_13 (.clk(and_1_out), .D(D4), .Q(d_ff_13_q));  // open: Qn, preset, en, reset
  D_Flip_Flop #(.trigger("high")) d_ff_14 (.clk(and_1_out), .D(D5), .Q(d_ff_14_q));  // open: Qn, preset, en, reset
  D_Flip_Flop #(.trigger("high")) d_ff_15 (.clk(and_1_out), .D(D6), .Q(d_ff_15_q));  // open: Qn, preset, en, reset
  D_Flip_Flop #(.trigger("high")) d_ff_16 (.clk(and_1_out), .D(D7), .Q(d_ff_16_q));  // open: Qn, preset, en, reset
  Multiplexer #(.enable("false")) multiplexer_1 (.in0(d_ff_1_qn), .in1(d_ff_1_q), .out(multiplexer_1_out), .sel(1'b1));
  Multiplexer #(.enable("false")) multiplexer_2 (
    .in0(d_ff_2_qn), .in1(d_ff_2_q), .out(multiplexer_2_out), .sel(nor_1_out));
  Multiplexer #(.enable("false")) multiplexer_3 (
    .in0(d_ff_3_qn), .in1(d_ff_3_q), .out(multiplexer_3_out), .sel(nor_2_out));
  Multiplexer #(.enable("false")) multiplexer_4 (
    .in0(d_ff_4_qn), .in1(d_ff_4_q), .out(multiplexer_4_out), .sel(nor_3_out));
  Multiplexer #(.enable("false")) multiplexer_5 (
    .in0(d_ff_5_qn), .in1(d_ff_5_q), .out(multiplexer_5_out), .sel(nor_4_out));
  Multiplexer #(.enable("false")) multiplexer_6 (
    .in0(d_ff_6_qn), .in1(d_ff_6_q), .out(multiplexer_6_out), .sel(nor_5_out));
  Multiplexer #(.enable("false")) multiplexer_7 (
    .in0(d_ff_7_qn), .in1(d_ff_7_q), .out(multiplexer_7_out), .sel(nor_6_out));
  Multiplexer #(.enable("false")) multiplexer_8 (
    .in0(d_ff_8_qn), .in1(d_ff_8_q), .out(multiplexer_8_out), .sel(nor_7_out));
  D_Flip_Flop d_ff_17 (.clk(nACLK), .D(multiplexer_1_out), .Qn(d_ff_17_qn));  // open: Q, preset, en, reset
  not not_1 (not_1_out, 1'b1);
  D_Flip_Flop d_ff_18 (.clk(nACLK), .D(multiplexer_2_out), .Qn(d_ff_18_qn));  // open: Q, preset, en, reset
  not not_2 (not_2_out, nor_1_out);
  D_Flip_Flop d_ff_19 (.clk(nACLK), .D(multiplexer_3_out), .Qn(d_ff_19_qn));  // open: Q, preset, en, reset
  not not_3 (not_3_out, nor_2_out);
  D_Flip_Flop d_ff_20 (.clk(nACLK), .D(multiplexer_4_out), .Qn(d_ff_20_qn));  // open: Q, preset, en, reset
  not not_4 (not_4_out, nor_3_out);
  D_Flip_Flop d_ff_21 (.clk(nACLK), .D(multiplexer_5_out), .Qn(d_ff_21_qn));  // open: Q, preset, en, reset
  not not_5 (not_5_out, nor_4_out);
  D_Flip_Flop d_ff_22 (.clk(nACLK), .D(multiplexer_6_out), .Qn(d_ff_22_qn));  // open: Q, preset, en, reset
  not not_6 (not_6_out, nor_5_out);
  D_Flip_Flop d_ff_23 (.clk(nACLK), .D(multiplexer_7_out), .Qn(d_ff_23_qn));  // open: Q, preset, en, reset
  not not_7 (not_7_out, nor_6_out);
  D_Flip_Flop d_ff_24 (.clk(nACLK), .D(multiplexer_8_out), .Qn(d_ff_24_qn));  // open: Q, preset, en, reset
  not not_8 (not_8_out, nor_7_out);
  nor nor_1 (nor_1_out, d_ff_1_qn, not_1_out);
  nor nor_2 (nor_2_out, d_ff_2_qn, not_2_out);
  nor nor_3 (nor_3_out, d_ff_3_qn, not_3_out);
  nor nor_4 (nor_4_out, d_ff_4_qn, not_4_out);
  nor nor_5 (nor_5_out, d_ff_5_qn, not_5_out);
  nor nor_6 (nor_6_out, d_ff_6_qn, not_6_out);
  nor nor_7 (nor_7_out, d_ff_7_qn, not_7_out);
  nor nor_8 (SPRE, d_ff_8_qn, not_8_out);
  Multiplexer #(.enable("false")) multiplexer_9 (.in0(d_ff_1_q), .in1(1'b0), .out(SPRA0), .sel(SPR_PPU));
  Multiplexer #(.enable("false")) multiplexer_10 (.in0(d_ff_2_q), .in1(1'b0), .out(SPRA1), .sel(SPR_PPU));
  Multiplexer #(.enable("false")) multiplexer_11 (.in0(d_ff_3_q), .in1(1'b1), .out(SPRA2), .sel(SPR_PPU));
  Multiplexer #(.enable("false")) multiplexer_12 (.in0(d_ff_4_q), .in1(1'b0), .out(SPRA3), .sel(SPR_PPU));
  Multiplexer #(.enable("false")) multiplexer_13 (.in0(d_ff_5_q), .in1(1'b0), .out(SPRA4), .sel(SPR_PPU));
  Multiplexer #(.enable("false")) multiplexer_14 (.in0(d_ff_6_q), .in1(1'b0), .out(SPRA5), .sel(SPR_PPU));
  Multiplexer #(.enable("false")) multiplexer_15 (.in0(d_ff_7_q), .in1(1'b0), .out(SPRA6), .sel(SPR_PPU));
  Multiplexer #(.enable("false")) multiplexer_16 (.in0(d_ff_8_q), .in1(1'b0), .out(SPRA7), .sel(SPR_PPU));
  Multiplexer #(.enable("false")) multiplexer_17 (.in0(d_ff_9_q), .in1(1'b0), .out(SPRA8), .sel(SPR_PPU));
  Multiplexer #(.enable("false")) multiplexer_18 (.in0(d_ff_10_q), .in1(1'b0), .out(SPRA9), .sel(SPR_PPU));
  Multiplexer #(.enable("false")) multiplexer_19 (.in0(d_ff_11_q), .in1(1'b0), .out(SPRA10), .sel(SPR_PPU));
  Multiplexer #(.enable("false")) multiplexer_20 (.in0(d_ff_12_q), .in1(1'b0), .out(SPRA11), .sel(SPR_PPU));
  Multiplexer #(.enable("false")) multiplexer_21 (.in0(d_ff_13_q), .in1(1'b0), .out(SPRA12), .sel(SPR_PPU));
  Multiplexer #(.enable("false")) multiplexer_22 (.in0(d_ff_14_q), .in1(1'b1), .out(SPRA13), .sel(SPR_PPU));
  Multiplexer #(.enable("false")) multiplexer_23 (.in0(d_ff_15_q), .in1(1'b0), .out(SPRA14), .sel(SPR_PPU));
  Multiplexer #(.enable("false")) multiplexer_24 (.in0(d_ff_16_q), .in1(1'b0), .out(SPRA15), .sel(SPR_PPU));
endmodule

// DMA CONTROL
module DMA_CONTROL (
  input  ACLK,
  input  PHI1,
  input  nACLK,
  input  W4014,
  input  SPRE,
  input  RUNDMC,
  input  in_7,
  input  R_W,
  input  RES,
  output SPRS,
  output RDY,
  output SPR_PPU,
  output SPR_CPU
);

  wire and_1_out, d_ff_1_q, d_ff_2_q, d_ff_3_qn, nand_1_out, nand_2_out, nor_1_out, nor_2_out, nor_4_out,
       nor_5_out, nor_6_out, nor_9_out, nor_10_out, nor_11_out, not_1_out, not_2_out, not_3_out, not_4_out;

  not not_1 (not_1_out, ACLK);
  not not_2 (not_2_out, PHI1);
  D_Flip_Flop d_ff_1 (.clk(nACLK), .D(SPRE), .Q(d_ff_1_q));  // open: Qn, preset, en, reset
  not not_3 (not_3_out, not_1_out);
  D_Flip_Flop d_ff_2 (.clk(not_1_out), .D(nor_5_out), .Q(d_ff_2_q));  // open: Qn, preset, en, reset
  nand nand_1 (nand_1_out, R_W, not_2_out);
  nor nor_1 (nor_1_out, not_1_out, nor_2_out);
  nor nor_2 (nor_2_out, nor_1_out, nACLK);
  and and_1 (and_1_out, d_ff_1_q, SPRS);
  nor nor_3 (SPRS, not_3_out, RUNDMC, d_ff_3_qn);
  not not_4 (not_4_out, d_ff_3_qn);
  nor nor_4 (nor_4_out, not_4_out, RES, nor_5_out);
  nor nor_5 (nor_5_out, W4014, nor_4_out);
  nor nor_6 (nor_6_out, d_ff_2_q, nand_1_out);
  nor nor_7 (SPR_PPU, RUNDMC, d_ff_3_qn, nor_1_out);
  nor nor_8 (SPR_CPU, RUNDMC, d_ff_3_qn, nor_2_out);
  nor nor_9 (nor_9_out, and_1_out, RES, nor_10_out);
  nor nor_10 (nor_10_out, nor_9_out, nor_6_out);
  nor nor_11 (nor_11_out, not_4_out, nor_4_out);
  D_Flip_Flop d_ff_3 (.clk(nACLK), .D(nor_9_out), .Qn(d_ff_3_qn));  // open: Q, preset, en, reset
  nand nand_2 (nand_2_out, nor_11_out, in_7);
  not not_5 (RDY, nand_2_out);

  // Notes on the sheet:
  //   /ACLK2
  //   INV2
  //   DL2
  //   INV4
  //   INV3
  //   DL1
  //   NAND2
  //   NORFF1
  //   RS3
  //   NORFF2
  //   NOR6
  //   NORFF1
  //   RS2
  //   NORFF2
  //   NORFF1
  //   RS1
  //   NORFF2
  //   NOR4
  //   NOR2
  //   NOR3
  //   DL3
  //   NOR5
endmodule

module DMA_ADDRESS_MUX (
  input  SPR_PPU,
  input  SPR_CPU,
  input  Z4,
  input  SPRA0,
  input  CPUA0,
  input  DMC0,
  input  SPRA1,
  input  CPUA1,
  input  DMC1,
  input  SPRA2,
  input  CPUA2,
  input  DMC2,
  input  SPRA3,
  input  CPUA3,
  input  DMC3,
  input  SPRA4,
  input  CPUA4,
  input  DMC4,
  input  SPRA5,
  input  CPUA5,
  input  DMC5,
  input  SPRA6,
  input  CPUA6,
  input  DMC6,
  input  SPRA7,
  input  CPUA7,
  input  DMC7,
  input  SPRA8,
  input  CPUA8,
  input  DMC8,
  input  SPRA9,
  input  CPUA9,
  input  DMC9,
  input  SPRA10,
  input  CPUA10,
  input  DMC10,
  input  SPRA11,
  input  CPUA11,
  input  DMC11,
  input  SPRA12,
  input  CPUA12,
  input  DMC12,
  input  SPRA13,
  input  CPUA13,
  input  DMC13,
  input  SPRA14,
  input  CPUA14,
  input  DMC14,
  input  SPRA15,
  input  CPUA15,
  output CPU_AB,
  output DMC_AB,
  output A0,
  output A1,
  output A2,
  output A3,
  output A4,
  output A5,
  output A6,
  output A7,
  output A8,
  output A9,
  output A10,
  output A11,
  output A12,
  output A13,
  output A14,
  output A15
);

  not not_1 (DMC_AB, Z4);
  nor nor_1 (CPU_AB, SPR_PPU, SPR_CPU, DMC_AB);
  Multiplexer #(.select(2), .enable("false")) multiplexer_1 (
    .in0(SPRA0), .in1(CPUA0), .in2(DMC0), .out(A0), .sel({DMC_AB, CPU_AB}));  // open: in3
  Multiplexer #(.select(2), .enable("false")) multiplexer_2 (
    .in0(SPRA1), .in1(CPUA1), .in2(DMC1), .out(A1), .sel({DMC_AB, CPU_AB}));  // open: in3
  Multiplexer #(.select(2), .enable("false")) multiplexer_3 (
    .in0(SPRA2), .in1(CPUA2), .in2(DMC2), .out(A2), .sel({DMC_AB, CPU_AB}));  // open: in3
  Multiplexer #(.select(2), .enable("false")) multiplexer_4 (
    .in0(SPRA3), .in1(CPUA3), .in2(DMC3), .out(A3), .sel({DMC_AB, CPU_AB}));  // open: in3
  Multiplexer #(.select(2), .enable("false")) multiplexer_5 (
    .in0(SPRA4), .in1(CPUA4), .in2(DMC4), .out(A4), .sel({DMC_AB, CPU_AB}));  // open: in3
  Multiplexer #(.select(2), .enable("false")) multiplexer_6 (
    .in0(SPRA5), .in1(CPUA5), .in2(DMC5), .out(A5), .sel({DMC_AB, CPU_AB}));  // open: in3
  Multiplexer #(.select(2), .enable("false")) multiplexer_7 (
    .in0(SPRA6), .in1(CPUA6), .in2(DMC6), .out(A6), .sel({DMC_AB, CPU_AB}));  // open: in3
  Multiplexer #(.select(2), .enable("false")) multiplexer_8 (
    .in0(SPRA7), .in1(CPUA7), .in2(DMC7), .out(A7), .sel({DMC_AB, CPU_AB}));  // open: in3
  Multiplexer #(.select(2), .enable("false")) multiplexer_9 (
    .in0(SPRA8), .in1(CPUA8), .in2(DMC8), .out(A8), .sel({DMC_AB, CPU_AB}));  // open: in3
  Multiplexer #(.select(2), .enable("false")) multiplexer_10 (
    .in0(SPRA9), .in1(CPUA9), .in2(DMC9), .out(A9), .sel({DMC_AB, CPU_AB}));  // open: in3
  Multiplexer #(.select(2), .enable("false")) multiplexer_11 (
    .in0(SPRA10), .in1(CPUA10), .in2(DMC10), .out(A10), .sel({DMC_AB, CPU_AB}));  // open: in3
  Multiplexer #(.select(2), .enable("false")) multiplexer_12 (
    .in0(SPRA11), .in1(CPUA11), .in2(DMC11), .out(A11), .sel({DMC_AB, CPU_AB}));  // open: in3
  Multiplexer #(.select(2), .enable("false")) multiplexer_13 (
    .in0(SPRA12), .in1(CPUA12), .in2(DMC12), .out(A12), .sel({DMC_AB, CPU_AB}));  // open: in3
  Multiplexer #(.select(2), .enable("false")) multiplexer_14 (
    .in0(SPRA13), .in1(CPUA13), .in2(DMC13), .out(A13), .sel({DMC_AB, CPU_AB}));  // open: in3
  Multiplexer #(.select(2), .enable("false")) multiplexer_15 (
    .in0(SPRA14), .in1(CPUA14), .in2(DMC14), .out(A14), .sel({DMC_AB, CPU_AB}));  // open: in3
  Multiplexer #(.select(2), .enable("false")) multiplexer_16 (
    .in0(SPRA15), .in1(CPUA15), .in2(1'b1), .out(A15), .sel({DMC_AB, CPU_AB}));  // open: in3

  // Notes on the sheet:
  //   INV1
  //   NOR1
endmodule

module DMA_BUFFER (
  input  nR4015,
  input  R_W,
  input  PHI2,
  input  SPR_CPU,
  input  SPR_PPU,
  input  D0I,
  input  D1I,
  input  D2I,
  input  D3I,
  input  D4I,
  input  D5I,
  input  D6I,
  input  D7I,
  output WR,
  output _2R_W,
  output D0O,
  output D1O,
  output D2O,
  output D3O,
  output D4O,
  output D5O,
  output D6O,
  output D7O
);

  wire d_ff_1_qn, d_ff_2_qn, d_ff_3_qn, d_ff_4_qn, d_ff_5_qn, d_ff_6_qn, d_ff_7_qn, d_ff_8_qn, not_1_out;

  not not_1 (not_1_out, R_W);
  nor nor_1 (_2R_W, not_1_out, SPR_PPU);
  D_Flip_Flop d_ff_1 (.clk(PHI2), .D(D0I), .Qn(d_ff_1_qn), .en(SPR_CPU));  // open: Q, preset, reset
  assign D0O = SPR_PPU ? ~d_ff_1_qn : 1'bz;  // Controlled_Inverter controlled_inverter_1
  nand nand_1 (WR, nR4015, _2R_W);
  D_Flip_Flop d_ff_2 (.clk(PHI2), .D(D1I), .Qn(d_ff_2_qn), .en(SPR_CPU));  // open: Q, preset, reset
  assign D1O = SPR_PPU ? ~d_ff_2_qn : 1'bz;  // Controlled_Inverter controlled_inverter_2
  D_Flip_Flop d_ff_3 (.clk(PHI2), .D(D2I), .Qn(d_ff_3_qn), .en(SPR_CPU));  // open: Q, preset, reset
  assign D2O = SPR_PPU ? ~d_ff_3_qn : 1'bz;  // Controlled_Inverter controlled_inverter_3
  D_Flip_Flop d_ff_4 (.clk(PHI2), .D(D3I), .Qn(d_ff_4_qn), .en(SPR_CPU));  // open: Q, preset, reset
  assign D3O = SPR_PPU ? ~d_ff_4_qn : 1'bz;  // Controlled_Inverter controlled_inverter_4
  D_Flip_Flop d_ff_5 (.clk(PHI2), .D(D4I), .Qn(d_ff_5_qn), .en(SPR_CPU));  // open: Q, preset, reset
  assign D4O = SPR_PPU ? ~d_ff_5_qn : 1'bz;  // Controlled_Inverter controlled_inverter_5
  D_Flip_Flop d_ff_6 (.clk(PHI2), .D(D5I), .Qn(d_ff_6_qn), .en(SPR_CPU));  // open: Q, preset, reset
  assign D5O = SPR_PPU ? ~d_ff_6_qn : 1'bz;  // Controlled_Inverter controlled_inverter_6
  D_Flip_Flop d_ff_7 (.clk(PHI2), .D(D6I), .Qn(d_ff_7_qn), .en(SPR_CPU));  // open: Q, preset, reset
  assign D6O = SPR_PPU ? ~d_ff_7_qn : 1'bz;  // Controlled_Inverter controlled_inverter_7
  D_Flip_Flop d_ff_8 (.clk(PHI2), .D(D7I), .Qn(d_ff_8_qn), .en(SPR_CPU));  // open: Q, preset, reset
  assign D7O = SPR_PPU ? ~d_ff_8_qn : 1'bz;  // Controlled_Inverter controlled_inverter_8

  // Notes on the sheet:
  //   INV1
  //   NOR1
endmodule

// LENGHT DECODER
module LENGHT_DECODER (
  input  D3,
  input  D4,
  input  D5,
  input  D6,
  input  D7,
  output LC7,
  output LC6,
  output LC5,
  output LC4,
  output LC3,
  output LC2,
  output LC1,
  output LC0
);

  wire not_1_out, not_2_out, not_3_out, not_4_out, not_5_out, transistor_138_out, transistor_139_out,
       transistor_140_out, transistor_141_out, transistor_142_out, transistor_143_out, transistor_144_out,
       transistor_145_out, transistor_146_out, transistor_147_out, transistor_148_out, transistor_149_out,
       transistor_150_out, transistor_151_out, transistor_152_out, transistor_153_out, transistor_162_out,
       transistor_164_out, transistor_165_out, transistor_167_out, transistor_168_out, transistor_170_out,
       transistor_171_out, transistor_173_out, transistor_174_out, transistor_176_out, transistor_177_out,
       transistor_179_out, transistor_180_out, transistor_182_out, transistor_183_out, transistor_185_out;

  Pull_Resistor #(.pull(1)) pull_resistor_1 (.node(LC0));
  Pull_Resistor #(.pull(1)) pull_resistor_2 (.node(LC1));
  Transistor #(.\type ("n")) transistor_1 (.in(1'b0), .out(LC1), .gate(transistor_138_out));
  Transistor #(.\type ("n")) transistor_2 (.in(1'b0), .out(LC1), .gate(transistor_140_out));
  Transistor #(.\type ("n")) transistor_3 (.in(1'b0), .out(LC1), .gate(transistor_142_out));
  Transistor #(.\type ("n")) transistor_4 (.in(1'b0), .out(LC1), .gate(transistor_144_out));
  Transistor #(.\type ("n")) transistor_5 (.in(1'b0), .out(LC1), .gate(transistor_146_out));
  Transistor #(.\type ("n")) transistor_6 (.in(1'b0), .out(LC1), .gate(transistor_148_out));
  Transistor #(.\type ("n")) transistor_7 (.in(1'b0), .out(LC1), .gate(transistor_150_out));
  Transistor #(.\type ("n")) transistor_8 (.in(1'b0), .out(LC1), .gate(transistor_152_out));
  Transistor #(.\type ("n")) transistor_9 (.in(1'b0), .out(LC1), .gate(transistor_153_out));
  Transistor #(.\type ("n")) transistor_10 (.in(1'b0), .out(LC1), .gate(transistor_174_out));
  Transistor #(.\type ("n")) transistor_11 (.in(1'b0), .out(LC1), .gate(transistor_176_out));
  Transistor #(.\type ("n")) transistor_12 (.in(1'b0), .out(LC1), .gate(transistor_185_out));
  Pull_Resistor #(.pull(1)) pull_resistor_3 (.node(LC2));
  Transistor #(.\type ("n")) transistor_13 (.in(1'b0), .out(LC2), .gate(transistor_139_out));
  Transistor #(.\type ("n")) transistor_14 (.in(1'b0), .out(LC2), .gate(transistor_140_out));
  Transistor #(.\type ("n")) transistor_15 (.in(1'b0), .out(LC2), .gate(transistor_143_out));
  Transistor #(.\type ("n")) transistor_16 (.in(1'b0), .out(LC2), .gate(transistor_144_out));
  Transistor #(.\type ("n")) transistor_17 (.in(1'b0), .out(LC2), .gate(transistor_147_out));
  Transistor #(.\type ("n")) transistor_18 (.in(1'b0), .out(LC2), .gate(transistor_148_out));
  Transistor #(.\type ("n")) transistor_19 (.in(1'b0), .out(LC2), .gate(transistor_151_out));
  Transistor #(.\type ("n")) transistor_20 (.in(1'b0), .out(LC2), .gate(transistor_152_out));
  Transistor #(.\type ("n")) transistor_21 (.in(1'b0), .out(LC2), .gate(transistor_173_out));
  Transistor #(.\type ("n")) transistor_22 (.in(1'b0), .out(LC2), .gate(transistor_174_out));
  Transistor #(.\type ("n")) transistor_23 (.in(1'b0), .out(LC2), .gate(transistor_177_out));
  Transistor #(.\type ("n")) transistor_24 (.in(1'b0), .out(LC2), .gate(transistor_183_out));
  Transistor #(.\type ("n")) transistor_25 (.in(1'b0), .out(LC2), .gate(transistor_185_out));
  Pull_Resistor #(.pull(1)) pull_resistor_4 (.node(LC3));
  Transistor #(.\type ("n")) transistor_26 (.in(1'b0), .out(LC3), .gate(transistor_141_out));
  Transistor #(.\type ("n")) transistor_27 (.in(1'b0), .out(LC3), .gate(transistor_142_out));
  Transistor #(.\type ("n")) transistor_28 (.in(1'b0), .out(LC3), .gate(transistor_143_out));
  Transistor #(.\type ("n")) transistor_29 (.in(1'b0), .out(LC3), .gate(transistor_144_out));
  Transistor #(.\type ("n")) transistor_30 (.in(1'b0), .out(LC3), .gate(transistor_149_out));
  Transistor #(.\type ("n")) transistor_31 (.in(1'b0), .out(LC3), .gate(transistor_150_out));
  Transistor #(.\type ("n")) transistor_32 (.in(1'b0), .out(LC3), .gate(transistor_151_out));
  Transistor #(.\type ("n")) transistor_33 (.in(1'b0), .out(LC3), .gate(transistor_152_out));
  Transistor #(.\type ("n")) transistor_34 (.in(1'b0), .out(LC3), .gate(transistor_165_out));
  Transistor #(.\type ("n")) transistor_35 (.in(1'b0), .out(LC3), .gate(transistor_171_out));
  Transistor #(.\type ("n")) transistor_36 (.in(1'b0), .out(LC3), .gate(transistor_182_out));
  Transistor #(.\type ("n")) transistor_37 (.in(1'b0), .out(LC3), .gate(transistor_183_out));
  Pull_Resistor #(.pull(1)) pull_resistor_5 (.node(LC4));
  Transistor #(.\type ("n")) transistor_38 (.in(1'b0), .out(LC4), .gate(transistor_145_out));
  Transistor #(.\type ("n")) transistor_39 (.in(1'b0), .out(LC4), .gate(transistor_146_out));
  Transistor #(.\type ("n")) transistor_40 (.in(1'b0), .out(LC4), .gate(transistor_147_out));
  Transistor #(.\type ("n")) transistor_41 (.in(1'b0), .out(LC4), .gate(transistor_148_out));
  Transistor #(.\type ("n")) transistor_42 (.in(1'b0), .out(LC4), .gate(transistor_149_out));
  Transistor #(.\type ("n")) transistor_43 (.in(1'b0), .out(LC4), .gate(transistor_150_out));
  Transistor #(.\type ("n")) transistor_44 (.in(1'b0), .out(LC4), .gate(transistor_151_out));
  Transistor #(.\type ("n")) transistor_45 (.in(1'b0), .out(LC4), .gate(transistor_152_out));
  Transistor #(.\type ("n")) transistor_46 (.in(1'b0), .out(LC4), .gate(transistor_164_out));
  Transistor #(.\type ("n")) transistor_47 (.in(1'b0), .out(LC4), .gate(transistor_165_out));
  Transistor #(.\type ("n")) transistor_48 (.in(1'b0), .out(LC4), .gate(transistor_170_out));
  Transistor #(.\type ("n")) transistor_49 (.in(1'b0), .out(LC4), .gate(transistor_173_out));
  Transistor #(.\type ("n")) transistor_50 (.in(1'b0), .out(LC4), .gate(transistor_176_out));
  Transistor #(.\type ("n")) transistor_51 (.in(1'b0), .out(LC4), .gate(transistor_180_out));
  Transistor #(.\type ("n")) transistor_52 (.in(1'b0), .out(LC4), .gate(transistor_182_out));
  Transistor #(.\type ("n")) transistor_53 (.in(1'b0), .out(LC4), .gate(transistor_185_out));
  Pull_Resistor #(.pull(1)) pull_resistor_6 (.node(LC5));
  Transistor #(.\type ("n")) transistor_54 (.in(1'b0), .out(LC5), .gate(transistor_138_out));
  Transistor #(.\type ("n")) transistor_55 (.in(1'b0), .out(LC5), .gate(transistor_139_out));
  Transistor #(.\type ("n")) transistor_56 (.in(1'b0), .out(LC5), .gate(transistor_140_out));
  Transistor #(.\type ("n")) transistor_57 (.in(1'b0), .out(LC5), .gate(transistor_141_out));
  Transistor #(.\type ("n")) transistor_58 (.in(1'b0), .out(LC5), .gate(transistor_142_out));
  Transistor #(.\type ("n")) transistor_59 (.in(1'b0), .out(LC5), .gate(transistor_143_out));
  Transistor #(.\type ("n")) transistor_60 (.in(1'b0), .out(LC5), .gate(transistor_144_out));
  Transistor #(.\type ("n")) transistor_61 (.in(1'b0), .out(LC5), .gate(transistor_145_out));
  Transistor #(.\type ("n")) transistor_62 (.in(1'b0), .out(LC5), .gate(transistor_146_out));
  Transistor #(.\type ("n")) transistor_63 (.in(1'b0), .out(LC5), .gate(transistor_147_out));
  Transistor #(.\type ("n")) transistor_64 (.in(1'b0), .out(LC5), .gate(transistor_148_out));
  Transistor #(.\type ("n")) transistor_65 (.in(1'b0), .out(LC5), .gate(transistor_149_out));
  Transistor #(.\type ("n")) transistor_66 (.in(1'b0), .out(LC5), .gate(transistor_150_out));
  Transistor #(.\type ("n")) transistor_67 (.in(1'b0), .out(LC5), .gate(transistor_151_out));
  Transistor #(.\type ("n")) transistor_68 (.in(1'b0), .out(LC5), .gate(transistor_152_out));
  Transistor #(.\type ("n")) transistor_69 (.in(1'b0), .out(LC5), .gate(transistor_162_out));
  Transistor #(.\type ("n")) transistor_70 (.in(1'b0), .out(LC5), .gate(transistor_164_out));
  Transistor #(.\type ("n")) transistor_71 (.in(1'b0), .out(LC5), .gate(transistor_165_out));
  Transistor #(.\type ("n")) transistor_72 (.in(1'b0), .out(LC5), .gate(transistor_168_out));
  Transistor #(.\type ("n")) transistor_73 (.in(1'b0), .out(LC5), .gate(transistor_171_out));
  Transistor #(.\type ("n")) transistor_74 (.in(1'b0), .out(LC5), .gate(transistor_173_out));
  Transistor #(.\type ("n")) transistor_75 (.in(1'b0), .out(LC5), .gate(transistor_174_out));
  Transistor #(.\type ("n")) transistor_76 (.in(1'b0), .out(LC5), .gate(transistor_176_out));
  Transistor #(.\type ("n")) transistor_77 (.in(1'b0), .out(LC5), .gate(transistor_179_out));
  Transistor #(.\type ("n")) transistor_78 (.in(1'b0), .out(LC5), .gate(transistor_180_out));
  Transistor #(.\type ("n")) transistor_79 (.in(1'b0), .out(LC5), .gate(transistor_183_out));
  Transistor #(.\type ("n")) transistor_80 (.in(1'b0), .out(LC5), .gate(transistor_185_out));
  Pull_Resistor #(.pull(1)) pull_resistor_7 (.node(LC6));
  Transistor #(.\type ("n")) transistor_81 (.in(1'b0), .out(LC6), .gate(transistor_138_out));
  Transistor #(.\type ("n")) transistor_82 (.in(1'b0), .out(LC6), .gate(transistor_139_out));
  Transistor #(.\type ("n")) transistor_83 (.in(1'b0), .out(LC6), .gate(transistor_140_out));
  Transistor #(.\type ("n")) transistor_84 (.in(1'b0), .out(LC6), .gate(transistor_141_out));
  Transistor #(.\type ("n")) transistor_85 (.in(1'b0), .out(LC6), .gate(transistor_142_out));
  Transistor #(.\type ("n")) transistor_86 (.in(1'b0), .out(LC6), .gate(transistor_143_out));
  Transistor #(.\type ("n")) transistor_87 (.in(1'b0), .out(LC6), .gate(transistor_144_out));
  Transistor #(.\type ("n")) transistor_88 (.in(1'b0), .out(LC6), .gate(transistor_145_out));
  Transistor #(.\type ("n")) transistor_89 (.in(1'b0), .out(LC6), .gate(transistor_146_out));
  Transistor #(.\type ("n")) transistor_90 (.in(1'b0), .out(LC6), .gate(transistor_147_out));
  Transistor #(.\type ("n")) transistor_91 (.in(1'b0), .out(LC6), .gate(transistor_148_out));
  Transistor #(.\type ("n")) transistor_92 (.in(1'b0), .out(LC6), .gate(transistor_149_out));
  Transistor #(.\type ("n")) transistor_93 (.in(1'b0), .out(LC6), .gate(transistor_150_out));
  Transistor #(.\type ("n")) transistor_94 (.in(1'b0), .out(LC6), .gate(transistor_151_out));
  Transistor #(.\type ("n")) transistor_95 (.in(1'b0), .out(LC6), .gate(transistor_152_out));
  Transistor #(.\type ("n")) transistor_96 (.in(1'b0), .out(LC6), .gate(transistor_162_out));
  Transistor #(.\type ("n")) transistor_97 (.in(1'b0), .out(LC6), .gate(transistor_164_out));
  Transistor #(.\type ("n")) transistor_98 (.in(1'b0), .out(LC6), .gate(transistor_167_out));
  Transistor #(.\type ("n")) transistor_99 (.in(1'b0), .out(LC6), .gate(transistor_170_out));
  Transistor #(.\type ("n")) transistor_100 (.in(1'b0), .out(LC6), .gate(transistor_171_out));
  Transistor #(.\type ("n")) transistor_101 (.in(1'b0), .out(LC6), .gate(transistor_173_out));
  Transistor #(.\type ("n")) transistor_102 (.in(1'b0), .out(LC6), .gate(transistor_174_out));
  Transistor #(.\type ("n")) transistor_103 (.in(1'b0), .out(LC6), .gate(transistor_176_out));
  Transistor #(.\type ("n")) transistor_104 (.in(1'b0), .out(LC6), .gate(transistor_177_out));
  Transistor #(.\type ("n")) transistor_105 (.in(1'b0), .out(LC6), .gate(transistor_179_out));
  Transistor #(.\type ("n")) transistor_106 (.in(1'b0), .out(LC6), .gate(transistor_182_out));
  Transistor #(.\type ("n")) transistor_107 (.in(1'b0), .out(LC6), .gate(transistor_183_out));
  Transistor #(.\type ("n")) transistor_108 (.in(1'b0), .out(LC6), .gate(transistor_185_out));
  Pull_Resistor #(.pull(1)) pull_resistor_8 (.node(LC7));
  Transistor #(.\type ("n")) transistor_109 (.in(1'b0), .out(LC7), .gate(transistor_138_out));
  Transistor #(.\type ("n")) transistor_110 (.in(1'b0), .out(LC7), .gate(transistor_139_out));
  Transistor #(.\type ("n")) transistor_111 (.in(1'b0), .out(LC7), .gate(transistor_140_out));
  Transistor #(.\type ("n")) transistor_112 (.in(1'b0), .out(LC7), .gate(transistor_141_out));
  Transistor #(.\type ("n")) transistor_113 (.in(1'b0), .out(LC7), .gate(transistor_142_out));
  Transistor #(.\type ("n")) transistor_114 (.in(1'b0), .out(LC7), .gate(transistor_143_out));
  Transistor #(.\type ("n")) transistor_115 (.in(1'b0), .out(LC7), .gate(transistor_144_out));
  Transistor #(.\type ("n")) transistor_116 (.in(1'b0), .out(LC7), .gate(transistor_145_out));
  Transistor #(.\type ("n")) transistor_117 (.in(1'b0), .out(LC7), .gate(transistor_146_out));
  Transistor #(.\type ("n")) transistor_118 (.in(1'b0), .out(LC7), .gate(transistor_147_out));
  Transistor #(.\type ("n")) transistor_119 (.in(1'b0), .out(LC7), .gate(transistor_148_out));
  Transistor #(.\type ("n")) transistor_120 (.in(1'b0), .out(LC7), .gate(transistor_149_out));
  Transistor #(.\type ("n")) transistor_121 (.in(1'b0), .out(LC7), .gate(transistor_150_out));
  Transistor #(.\type ("n")) transistor_122 (.in(1'b0), .out(LC7), .gate(transistor_151_out));
  Transistor #(.\type ("n")) transistor_123 (.in(1'b0), .out(LC7), .gate(transistor_152_out));
  Transistor #(.\type ("n")) transistor_124 (.in(1'b0), .out(LC7), .gate(transistor_162_out));
  Transistor #(.\type ("n")) transistor_125 (.in(1'b0), .out(LC7), .gate(transistor_164_out));
  Transistor #(.\type ("n")) transistor_126 (.in(1'b0), .out(LC7), .gate(transistor_165_out));
  Transistor #(.\type ("n")) transistor_127 (.in(1'b0), .out(LC7), .gate(transistor_168_out));
  Transistor #(.\type ("n")) transistor_128 (.in(1'b0), .out(LC7), .gate(transistor_170_out));
  Transistor #(.\type ("n")) transistor_129 (.in(1'b0), .out(LC7), .gate(transistor_171_out));
  Transistor #(.\type ("n")) transistor_130 (.in(1'b0), .out(LC7), .gate(transistor_173_out));
  Transistor #(.\type ("n")) transistor_131 (.in(1'b0), .out(LC7), .gate(transistor_174_out));
  Transistor #(.\type ("n")) transistor_132 (.in(1'b0), .out(LC7), .gate(transistor_176_out));
  Transistor #(.\type ("n")) transistor_133 (.in(1'b0), .out(LC7), .gate(transistor_177_out));
  Transistor #(.\type ("n")) transistor_134 (.in(1'b0), .out(LC7), .gate(transistor_180_out));
  Transistor #(.\type ("n")) transistor_135 (.in(1'b0), .out(LC7), .gate(transistor_182_out));
  Transistor #(.\type ("n")) transistor_136 (.in(1'b0), .out(LC7), .gate(transistor_183_out));
  Transistor #(.\type ("n")) transistor_137 (.in(1'b0), .out(LC7), .gate(transistor_185_out));
  Transistor #(.\type ("n"), .gate("br")) transistor_138 (.in(1'b0), .out(transistor_138_out), .gate(not_1_out));
  Transistor #(.\type ("n"), .gate("br")) transistor_139 (.in(1'b0), .out(transistor_139_out), .gate(not_1_out));
  Transistor #(.\type ("n"), .gate("br")) transistor_140 (.in(1'b0), .out(transistor_140_out), .gate(not_1_out));
  Transistor #(.\type ("n"), .gate("br")) transistor_141 (.in(1'b0), .out(transistor_141_out), .gate(not_1_out));
  Transistor #(.\type ("n"), .gate("br")) transistor_142 (.in(1'b0), .out(transistor_142_out), .gate(not_1_out));
  Transistor #(.\type ("n"), .gate("br")) transistor_143 (.in(1'b0), .out(transistor_143_out), .gate(not_1_out));
  Transistor #(.\type ("n"), .gate("br")) transistor_144 (.in(1'b0), .out(transistor_144_out), .gate(not_1_out));
  Transistor #(.\type ("n"), .gate("br")) transistor_145 (.in(1'b0), .out(transistor_145_out), .gate(not_1_out));
  Transistor #(.\type ("n"), .gate("br")) transistor_146 (.in(1'b0), .out(transistor_146_out), .gate(not_1_out));
  Transistor #(.\type ("n"), .gate("br")) transistor_147 (.in(1'b0), .out(transistor_147_out), .gate(not_1_out));
  Transistor #(.\type ("n"), .gate("br")) transistor_148 (.in(1'b0), .out(transistor_148_out), .gate(not_1_out));
  Transistor #(.\type ("n"), .gate("br")) transistor_149 (.in(1'b0), .out(transistor_149_out), .gate(not_1_out));
  Transistor #(.\type ("n"), .gate("br")) transistor_150 (.in(1'b0), .out(transistor_150_out), .gate(not_1_out));
  Transistor #(.\type ("n"), .gate("br")) transistor_151 (.in(1'b0), .out(transistor_151_out), .gate(not_1_out));
  Transistor #(.\type ("n"), .gate("br")) transistor_152 (.in(1'b0), .out(transistor_152_out), .gate(not_1_out));
  Transistor #(.\type ("n"), .gate("br")) transistor_153 (.in(1'b0), .out(transistor_153_out), .gate(not_1_out));
  not not_1 (not_1_out, D3);
  Transistor #(.\type ("n"), .gate("br")) transistor_154 (.in(1'b0), .out(transistor_138_out), .gate(not_2_out));
  Transistor #(.\type ("n"), .gate("br")) transistor_155 (.in(1'b0), .out(transistor_140_out), .gate(not_2_out));
  Transistor #(.\type ("n"), .gate("br")) transistor_156 (.in(1'b0), .out(transistor_142_out), .gate(not_2_out));
  Transistor #(.\type ("n"), .gate("br")) transistor_157 (.in(1'b0), .out(transistor_144_out), .gate(not_2_out));
  Transistor #(.\type ("n"), .gate("br")) transistor_158 (.in(1'b0), .out(transistor_146_out), .gate(not_2_out));
  Transistor #(.\type ("n"), .gate("br")) transistor_159 (.in(1'b0), .out(transistor_148_out), .gate(not_2_out));
  Transistor #(.\type ("n"), .gate("br")) transistor_160 (.in(1'b0), .out(transistor_150_out), .gate(not_2_out));
  Transistor #(.\type ("n"), .gate("br")) transistor_161 (.in(1'b0), .out(transistor_152_out), .gate(not_2_out));
  Transistor #(.\type ("n"), .gate("br")) transistor_162 (.in(1'b0), .out(transistor_162_out), .gate(not_2_out));
  Transistor #(.\type ("n"), .gate("br")) transistor_163 (.in(1'b0), .out(transistor_162_out), .gate(D3));
  Transistor #(.\type ("n"), .gate("br")) transistor_164 (.in(1'b0), .out(transistor_164_out), .gate(D3));
  Transistor #(.\type ("n"), .gate("br")) transistor_165 (.in(1'b0), .out(transistor_165_out), .gate(not_2_out));
  Transistor #(.\type ("n"), .gate("br")) transistor_166 (.in(1'b0), .out(transistor_165_out), .gate(D3));
  Transistor #(.\type ("n"), .gate("br")) transistor_167 (.in(1'b0), .out(transistor_167_out), .gate(D3));
  Transistor #(.\type ("n"), .gate("br")) transistor_168 (.in(1'b0), .out(transistor_168_out), .gate(D3));
  Transistor #(.\type ("n"), .gate("br")) transistor_169 (.in(1'b0), .out(transistor_168_out), .gate(not_2_out));
  Transistor #(.\type ("n"), .gate("br")) transistor_170 (.in(1'b0), .out(transistor_170_out), .gate(D3));
  Transistor #(.\type ("n"), .gate("br")) transistor_171 (.in(1'b0), .out(transistor_171_out), .gate(not_2_out));
  Transistor #(.\type ("n"), .gate("br")) transistor_172 (.in(1'b0), .out(transistor_171_out), .gate(D3));
  Transistor #(.\type ("n"), .gate("br")) transistor_173 (.in(1'b0), .out(transistor_173_out), .gate(D3));
  Transistor #(.\type ("n"), .gate("br")) transistor_174 (.in(1'b0), .out(transistor_174_out), .gate(D3));
  Transistor #(.\type ("n"), .gate("br")) transistor_175 (.in(1'b0), .out(transistor_174_out), .gate(not_2_out));
  Transistor #(.\type ("n"), .gate("br")) transistor_176 (.in(1'b0), .out(transistor_176_out), .gate(D3));
  Transistor #(.\type ("n"), .gate("br")) transistor_177 (.in(1'b0), .out(transistor_177_out), .gate(D3));
  Transistor #(.\type ("n"), .gate("br")) transistor_178 (.in(1'b0), .out(transistor_177_out), .gate(not_2_out));
  Transistor #(.\type ("n"), .gate("br")) transistor_179 (.in(1'b0), .out(transistor_179_out), .gate(D3));
  Transistor #(.\type ("n"), .gate("br")) transistor_180 (.in(1'b0), .out(transistor_180_out), .gate(not_2_out));
  Transistor #(.\type ("n"), .gate("br")) transistor_181 (.in(1'b0), .out(transistor_180_out), .gate(D3));
  Transistor #(.\type ("n"), .gate("br")) transistor_182 (.in(1'b0), .out(transistor_182_out), .gate(D3));
  Transistor #(.\type ("n"), .gate("br")) transistor_183 (.in(1'b0), .out(transistor_183_out), .gate(D3));
  Transistor #(.\type ("n"), .gate("br")) transistor_184 (.in(1'b0), .out(transistor_183_out), .gate(not_2_out));
  Transistor #(.\type ("n"), .gate("br")) transistor_185 (.in(1'b0), .out(transistor_185_out), .gate(D3));
  Transistor #(.\type ("n"), .gate("br")) transistor_186 (.in(1'b0), .out(transistor_139_out), .gate(D4));
  Transistor #(.\type ("n"), .gate("br")) transistor_187 (.in(1'b0), .out(transistor_141_out), .gate(D4));
  Transistor #(.\type ("n"), .gate("br")) transistor_188 (.in(1'b0), .out(transistor_143_out), .gate(D4));
  Transistor #(.\type ("n"), .gate("br")) transistor_189 (.in(1'b0), .out(transistor_145_out), .gate(D4));
  Transistor #(.\type ("n"), .gate("br")) transistor_190 (.in(1'b0), .out(transistor_147_out), .gate(D4));
  Transistor #(.\type ("n"), .gate("br")) transistor_191 (.in(1'b0), .out(transistor_149_out), .gate(D4));
  Transistor #(.\type ("n"), .gate("br")) transistor_192 (.in(1'b0), .out(transistor_151_out), .gate(D4));
  Transistor #(.\type ("n"), .gate("br")) transistor_193 (.in(1'b0), .out(transistor_153_out), .gate(D4));
  Transistor #(.\type ("n"), .gate("br")) transistor_194 (.in(1'b0), .out(transistor_164_out), .gate(D4));
  Transistor #(.\type ("n"), .gate("br")) transistor_195 (.in(1'b0), .out(transistor_167_out), .gate(D4));
  Transistor #(.\type ("n"), .gate("br")) transistor_196 (.in(1'b0), .out(transistor_170_out), .gate(D4));
  Transistor #(.\type ("n"), .gate("br")) transistor_197 (.in(1'b0), .out(transistor_173_out), .gate(D4));
  Transistor #(.\type ("n"), .gate("br")) transistor_198 (.in(1'b0), .out(transistor_176_out), .gate(D4));
  Transistor #(.\type ("n"), .gate("br")) transistor_199 (.in(1'b0), .out(transistor_179_out), .gate(D4));
  Transistor #(.\type ("n"), .gate("br")) transistor_200 (.in(1'b0), .out(transistor_182_out), .gate(D4));
  Transistor #(.\type ("n"), .gate("br")) transistor_201 (.in(1'b0), .out(transistor_185_out), .gate(D4));
  not not_2 (not_2_out, D4);
  Transistor #(.\type ("n"), .gate("br")) transistor_202 (.in(1'b0), .out(transistor_138_out), .gate(not_3_out));
  Transistor #(.\type ("n"), .gate("br")) transistor_203 (.in(1'b0), .out(transistor_139_out), .gate(not_3_out));
  Transistor #(.\type ("n"), .gate("br")) transistor_204 (.in(1'b0), .out(transistor_142_out), .gate(not_3_out));
  Transistor #(.\type ("n"), .gate("br")) transistor_205 (.in(1'b0), .out(transistor_143_out), .gate(not_3_out));
  Transistor #(.\type ("n"), .gate("br")) transistor_206 (.in(1'b0), .out(transistor_146_out), .gate(not_3_out));
  Transistor #(.\type ("n"), .gate("br")) transistor_207 (.in(1'b0), .out(transistor_147_out), .gate(not_3_out));
  Transistor #(.\type ("n"), .gate("br")) transistor_208 (.in(1'b0), .out(transistor_150_out), .gate(not_3_out));
  Transistor #(.\type ("n"), .gate("br")) transistor_209 (.in(1'b0), .out(transistor_151_out), .gate(not_3_out));
  Transistor #(.\type ("n"), .gate("br")) transistor_210 (.in(1'b0), .out(transistor_162_out), .gate(not_3_out));
  Transistor #(.\type ("n"), .gate("br")) transistor_211 (.in(1'b0), .out(transistor_164_out), .gate(not_3_out));
  Transistor #(.\type ("n"), .gate("br")) transistor_212 (.in(1'b0), .out(transistor_168_out), .gate(not_3_out));
  Transistor #(.\type ("n"), .gate("br")) transistor_213 (.in(1'b0), .out(transistor_170_out), .gate(not_3_out));
  Transistor #(.\type ("n"), .gate("br")) transistor_214 (.in(1'b0), .out(transistor_174_out), .gate(not_3_out));
  Transistor #(.\type ("n"), .gate("br")) transistor_215 (.in(1'b0), .out(transistor_176_out), .gate(not_3_out));
  Transistor #(.\type ("n"), .gate("br")) transistor_216 (.in(1'b0), .out(transistor_180_out), .gate(not_3_out));
  Transistor #(.\type ("n"), .gate("br")) transistor_217 (.in(1'b0), .out(transistor_182_out), .gate(not_3_out));
  Transistor #(.\type ("n"), .gate("br")) transistor_218 (.in(1'b0), .out(transistor_140_out), .gate(D5));
  Transistor #(.\type ("n"), .gate("br")) transistor_219 (.in(1'b0), .out(transistor_141_out), .gate(D5));
  Transistor #(.\type ("n"), .gate("br")) transistor_220 (.in(1'b0), .out(transistor_144_out), .gate(D5));
  Transistor #(.\type ("n"), .gate("br")) transistor_221 (.in(1'b0), .out(transistor_145_out), .gate(D5));
  Transistor #(.\type ("n"), .gate("br")) transistor_222 (.in(1'b0), .out(transistor_148_out), .gate(D5));
  Transistor #(.\type ("n"), .gate("br")) transistor_223 (.in(1'b0), .out(transistor_149_out), .gate(D5));
  Transistor #(.\type ("n"), .gate("br")) transistor_224 (.in(1'b0), .out(transistor_152_out), .gate(D5));
  Transistor #(.\type ("n"), .gate("br")) transistor_225 (.in(1'b0), .out(transistor_153_out), .gate(D5));
  Transistor #(.\type ("n"), .gate("br")) transistor_226 (.in(1'b0), .out(transistor_165_out), .gate(D5));
  Transistor #(.\type ("n"), .gate("br")) transistor_227 (.in(1'b0), .out(transistor_167_out), .gate(D5));
  Transistor #(.\type ("n"), .gate("br")) transistor_228 (.in(1'b0), .out(transistor_171_out), .gate(D5));
  Transistor #(.\type ("n"), .gate("br")) transistor_229 (.in(1'b0), .out(transistor_173_out), .gate(D5));
  Transistor #(.\type ("n"), .gate("br")) transistor_230 (.in(1'b0), .out(transistor_177_out), .gate(D5));
  Transistor #(.\type ("n"), .gate("br")) transistor_231 (.in(1'b0), .out(transistor_179_out), .gate(D5));
  Transistor #(.\type ("n"), .gate("br")) transistor_232 (.in(1'b0), .out(transistor_183_out), .gate(D5));
  Transistor #(.\type ("n"), .gate("br")) transistor_233 (.in(1'b0), .out(transistor_185_out), .gate(D5));
  not not_3 (not_3_out, D5);
  Transistor #(.\type ("n"), .gate("br")) transistor_234 (.in(1'b0), .out(transistor_138_out), .gate(not_4_out));
  Transistor #(.\type ("n"), .gate("br")) transistor_235 (.in(1'b0), .out(transistor_139_out), .gate(not_4_out));
  Transistor #(.\type ("n"), .gate("br")) transistor_236 (.in(1'b0), .out(transistor_140_out), .gate(not_4_out));
  Transistor #(.\type ("n"), .gate("br")) transistor_237 (.in(1'b0), .out(transistor_141_out), .gate(not_4_out));
  Transistor #(.\type ("n"), .gate("br")) transistor_238 (.in(1'b0), .out(transistor_146_out), .gate(not_4_out));
  Transistor #(.\type ("n"), .gate("br")) transistor_239 (.in(1'b0), .out(transistor_147_out), .gate(not_4_out));
  Transistor #(.\type ("n"), .gate("br")) transistor_240 (.in(1'b0), .out(transistor_148_out), .gate(not_4_out));
  Transistor #(.\type ("n"), .gate("br")) transistor_241 (.in(1'b0), .out(transistor_149_out), .gate(not_4_out));
  Transistor #(.\type ("n"), .gate("br")) transistor_242 (.in(1'b0), .out(transistor_162_out), .gate(not_4_out));
  Transistor #(.\type ("n"), .gate("br")) transistor_243 (.in(1'b0), .out(transistor_164_out), .gate(not_4_out));
  Transistor #(.\type ("n"), .gate("br")) transistor_244 (.in(1'b0), .out(transistor_165_out), .gate(not_4_out));
  Transistor #(.\type ("n"), .gate("br")) transistor_245 (.in(1'b0), .out(transistor_167_out), .gate(not_4_out));
  Transistor #(.\type ("n"), .gate("br")) transistor_246 (.in(1'b0), .out(transistor_174_out), .gate(not_4_out));
  Transistor #(.\type ("n"), .gate("br")) transistor_247 (.in(1'b0), .out(transistor_176_out), .gate(not_4_out));
  Transistor #(.\type ("n"), .gate("br")) transistor_248 (.in(1'b0), .out(transistor_177_out), .gate(not_4_out));
  Transistor #(.\type ("n"), .gate("br")) transistor_249 (.in(1'b0), .out(transistor_179_out), .gate(not_4_out));
  Transistor #(.\type ("n"), .gate("br")) transistor_250 (.in(1'b0), .out(transistor_142_out), .gate(D6));
  Transistor #(.\type ("n"), .gate("br")) transistor_251 (.in(1'b0), .out(transistor_143_out), .gate(D6));
  Transistor #(.\type ("n"), .gate("br")) transistor_252 (.in(1'b0), .out(transistor_144_out), .gate(D6));
  Transistor #(.\type ("n"), .gate("br")) transistor_253 (.in(1'b0), .out(transistor_145_out), .gate(D6));
  Transistor #(.\type ("n"), .gate("br")) transistor_254 (.in(1'b0), .out(transistor_150_out), .gate(D6));
  Transistor #(.\type ("n"), .gate("br")) transistor_255 (.in(1'b0), .out(transistor_151_out), .gate(D6));
  Transistor #(.\type ("n"), .gate("br")) transistor_256 (.in(1'b0), .out(transistor_152_out), .gate(D6));
  Transistor #(.\type ("n"), .gate("br")) transistor_257 (.in(1'b0), .out(transistor_153_out), .gate(D6));
  Transistor #(.\type ("n"), .gate("br")) transistor_258 (.in(1'b0), .out(transistor_168_out), .gate(D6));
  Transistor #(.\type ("n"), .gate("br")) transistor_259 (.in(1'b0), .out(transistor_170_out), .gate(D6));
  Transistor #(.\type ("n"), .gate("br")) transistor_260 (.in(1'b0), .out(transistor_171_out), .gate(D6));
  Transistor #(.\type ("n"), .gate("br")) transistor_261 (.in(1'b0), .out(transistor_173_out), .gate(D6));
  Transistor #(.\type ("n"), .gate("br")) transistor_262 (.in(1'b0), .out(transistor_180_out), .gate(D6));
  Transistor #(.\type ("n"), .gate("br")) transistor_263 (.in(1'b0), .out(transistor_182_out), .gate(D6));
  Transistor #(.\type ("n"), .gate("br")) transistor_264 (.in(1'b0), .out(transistor_183_out), .gate(D6));
  Transistor #(.\type ("n"), .gate("br")) transistor_265 (.in(1'b0), .out(transistor_185_out), .gate(D6));
  not not_4 (not_4_out, D6);
  Transistor #(.\type ("n"), .gate("br")) transistor_266 (.in(1'b0), .out(transistor_138_out), .gate(not_5_out));
  Transistor #(.\type ("n"), .gate("br")) transistor_267 (.in(1'b0), .out(transistor_139_out), .gate(not_5_out));
  Transistor #(.\type ("n"), .gate("br")) transistor_268 (.in(1'b0), .out(transistor_140_out), .gate(not_5_out));
  Transistor #(.\type ("n"), .gate("br")) transistor_269 (.in(1'b0), .out(transistor_141_out), .gate(not_5_out));
  Transistor #(.\type ("n"), .gate("br")) transistor_270 (.in(1'b0), .out(transistor_142_out), .gate(not_5_out));
  Transistor #(.\type ("n"), .gate("br")) transistor_271 (.in(1'b0), .out(transistor_143_out), .gate(not_5_out));
  Transistor #(.\type ("n"), .gate("br")) transistor_272 (.in(1'b0), .out(transistor_144_out), .gate(not_5_out));
  Transistor #(.\type ("n"), .gate("br")) transistor_273 (.in(1'b0), .out(transistor_145_out), .gate(not_5_out));
  Transistor #(.\type ("n"), .gate("br")) transistor_274 (.in(1'b0), .out(transistor_162_out), .gate(not_5_out));
  Transistor #(.\type ("n"), .gate("br")) transistor_275 (.in(1'b0), .out(transistor_164_out), .gate(not_5_out));
  Transistor #(.\type ("n"), .gate("br")) transistor_276 (.in(1'b0), .out(transistor_165_out), .gate(not_5_out));
  Transistor #(.\type ("n"), .gate("br")) transistor_277 (.in(1'b0), .out(transistor_167_out), .gate(not_5_out));
  Transistor #(.\type ("n"), .gate("br")) transistor_278 (.in(1'b0), .out(transistor_168_out), .gate(not_5_out));
  Transistor #(.\type ("n"), .gate("br")) transistor_279 (.in(1'b0), .out(transistor_170_out), .gate(not_5_out));
  Transistor #(.\type ("n"), .gate("br")) transistor_280 (.in(1'b0), .out(transistor_171_out), .gate(not_5_out));
  Transistor #(.\type ("n"), .gate("br")) transistor_281 (.in(1'b0), .out(transistor_173_out), .gate(not_5_out));
  not not_5 (not_5_out, D7);
  Pull_Resistor #(.pull(1)) pull_resistor_9 (.node(transistor_138_out));
  Pull_Resistor #(.pull(1)) pull_resistor_10 (.node(transistor_139_out));
  Pull_Resistor #(.pull(1)) pull_resistor_11 (.node(transistor_140_out));
  Pull_Resistor #(.pull(1)) pull_resistor_12 (.node(transistor_141_out));
  Pull_Resistor #(.pull(1)) pull_resistor_13 (.node(transistor_142_out));
  Pull_Resistor #(.pull(1)) pull_resistor_14 (.node(transistor_143_out));
  Pull_Resistor #(.pull(1)) pull_resistor_15 (.node(transistor_144_out));
  Pull_Resistor #(.pull(1)) pull_resistor_16 (.node(transistor_145_out));
  Pull_Resistor #(.pull(1)) pull_resistor_17 (.node(transistor_146_out));
  Transistor #(.\type ("n"), .gate("br")) transistor_282 (.in(1'b0), .out(transistor_146_out), .gate(D7));
  Transistor #(.\type ("n"), .gate("br")) transistor_283 (.in(1'b0), .out(transistor_147_out), .gate(D7));
  Pull_Resistor #(.pull(1)) pull_resistor_18 (.node(transistor_147_out));
  Pull_Resistor #(.pull(1)) pull_resistor_19 (.node(transistor_148_out));
  Transistor #(.\type ("n"), .gate("br")) transistor_284 (.in(1'b0), .out(transistor_148_out), .gate(D7));
  Transistor #(.\type ("n"), .gate("br")) transistor_285 (.in(1'b0), .out(transistor_149_out), .gate(D7));
  Pull_Resistor #(.pull(1)) pull_resistor_20 (.node(transistor_149_out));
  Pull_Resistor #(.pull(1)) pull_resistor_21 (.node(transistor_150_out));
  Transistor #(.\type ("n"), .gate("br")) transistor_286 (.in(1'b0), .out(transistor_150_out), .gate(D7));
  Transistor #(.\type ("n"), .gate("br")) transistor_287 (.in(1'b0), .out(transistor_151_out), .gate(D7));
  Pull_Resistor #(.pull(1)) pull_resistor_22 (.node(transistor_151_out));
  Transistor #(.\type ("n"), .gate("br")) transistor_288 (.in(1'b0), .out(transistor_152_out), .gate(D7));
  Pull_Resistor #(.pull(1)) pull_resistor_23 (.node(transistor_152_out));
  Pull_Resistor #(.pull(1)) pull_resistor_24 (.node(transistor_153_out));
  Transistor #(.\type ("n"), .gate("br")) transistor_289 (.in(1'b0), .out(transistor_153_out), .gate(D7));
  Pull_Resistor #(.pull(1)) pull_resistor_25 (.node(transistor_162_out));
  Pull_Resistor #(.pull(1)) pull_resistor_26 (.node(transistor_164_out));
  Pull_Resistor #(.pull(1)) pull_resistor_27 (.node(transistor_165_out));
  Pull_Resistor #(.pull(1)) pull_resistor_28 (.node(transistor_167_out));
  Pull_Resistor #(.pull(1)) pull_resistor_29 (.node(transistor_168_out));
  Pull_Resistor #(.pull(1)) pull_resistor_30 (.node(transistor_170_out));
  Pull_Resistor #(.pull(1)) pull_resistor_31 (.node(transistor_171_out));
  Pull_Resistor #(.pull(1)) pull_resistor_32 (.node(transistor_173_out));
  Transistor #(.\type ("n"), .gate("br")) transistor_290 (.in(1'b0), .out(transistor_174_out), .gate(D7));
  Pull_Resistor #(.pull(1)) pull_resistor_33 (.node(transistor_174_out));
  Pull_Resistor #(.pull(1)) pull_resistor_34 (.node(transistor_176_out));
  Transistor #(.\type ("n"), .gate("br")) transistor_291 (.in(1'b0), .out(transistor_176_out), .gate(D7));
  Pull_Resistor #(.pull(1)) pull_resistor_35 (.node(transistor_177_out));
  Transistor #(.\type ("n"), .gate("br")) transistor_292 (.in(1'b0), .out(transistor_177_out), .gate(D7));
  Transistor #(.\type ("n"), .gate("br")) transistor_293 (.in(1'b0), .out(transistor_179_out), .gate(D7));
  Pull_Resistor #(.pull(1)) pull_resistor_36 (.node(transistor_179_out));
  Transistor #(.\type ("n"), .gate("br")) transistor_294 (.in(1'b0), .out(transistor_180_out), .gate(D7));
  Pull_Resistor #(.pull(1)) pull_resistor_37 (.node(transistor_180_out));
  Transistor #(.\type ("n"), .gate("br")) transistor_295 (.in(1'b0), .out(transistor_182_out), .gate(D7));
  Pull_Resistor #(.pull(1)) pull_resistor_38 (.node(transistor_182_out));
  Transistor #(.\type ("n"), .gate("br")) transistor_296 (.in(1'b0), .out(transistor_183_out), .gate(D7));
  Pull_Resistor #(.pull(1)) pull_resistor_39 (.node(transistor_183_out));
  Transistor #(.\type ("n"), .gate("br")) transistor_297 (.in(1'b0), .out(transistor_185_out), .gate(D7));
  Pull_Resistor #(.pull(1)) pull_resistor_40 (.node(transistor_185_out));

  // Notes on the sheet:
  //   /D3
  //   D3
  //   /D4
  //   D4
  //   /D5
  //   D5
  //   /D6
  //   D6
  //   /D7
  //   D7
  //   8
  //   7
  //   6
  //   5
  //   4
  //   3
  //   2
  //   1
  //   8
  //   7
  //   6
  //   5
  //   4
  //   3
  //   2
  //   1
  //   8
  //   7
  //   6
  //   5
  //   4
  //   3
  //   2
  //   1
  //   8
  //   7
  //   6
  //   5
  //   4
  //   3
  //   2
  //   1
endmodule

// LENGHT COUNTER
module LENGHT_COUNTER (
  input  nACLK,
  input  STEP,
  input  W4003,
  input  LC7,
  input  RES,
  input  LC6,
  input  LC5,
  input  LC4,
  input  LC3,
  input  LC2,
  input  LC1,
  input  LC0,
  input  HALT,
  output Carry_Out
);

  wire and_1_out, and_2_out, and_3_out, and_4_out, and_5_out, and_6_out, and_7_out, and_8_out, and_9_out,
       and_10_out, and_11_out, and_12_out, and_13_out, and_14_out, and_15_out, and_16_out, d_ff_1_q,
       d_ff_1_qn, d_ff_2_q, d_ff_2_qn, d_ff_3_q, d_ff_3_qn, d_ff_4_q, d_ff_4_qn, d_ff_5_q, d_ff_5_qn,
       d_ff_6_q, d_ff_6_qn, d_ff_7_q, d_ff_7_qn, d_ff_8_q, d_ff_8_qn, d_ff_9_qn, d_ff_10_qn, d_ff_11_qn,
       d_ff_12_qn, d_ff_13_qn, d_ff_14_qn, d_ff_15_qn, d_ff_16_qn, multiplexer_1_out, multiplexer_2_out,
       multiplexer_3_out, multiplexer_4_out, multiplexer_5_out, multiplexer_6_out, multiplexer_7_out,
       multiplexer_8_out, nor_2_out, nor_3_out, nor_4_out, nor_5_out, nor_6_out, nor_7_out, nor_8_out,
       not_1_out, not_2_out, not_3_out, not_4_out, not_5_out, not_6_out, not_7_out, not_8_out, not_9_out,
       not_10_out, not_11_out, not_12_out, not_13_out, not_14_out, not_15_out, not_16_out, or_1_out,
       or_2_out, or_3_out, or_4_out, or_5_out, or_6_out, or_7_out, or_8_out;

  and and_1 (and_1_out, W4003, LC7);
  and and_2 (and_2_out, W4003, not_1_out);
  not not_1 (not_1_out, LC7);
  and and_3 (and_3_out, W4003, LC6);
  and and_4 (and_4_out, W4003, not_2_out);
  not not_2 (not_2_out, LC6);
  and and_5 (and_5_out, W4003, LC5);
  and and_6 (and_6_out, W4003, not_3_out);
  not not_3 (not_3_out, LC5);
  and and_7 (and_7_out, W4003, LC4);
  and and_8 (and_8_out, W4003, not_4_out);
  not not_4 (not_4_out, LC4);
  and and_9 (and_9_out, W4003, LC3);
  and and_10 (and_10_out, W4003, not_5_out);
  not not_5 (not_5_out, LC3);
  and and_11 (and_11_out, W4003, LC2);
  and and_12 (and_12_out, W4003, not_6_out);
  not not_6 (not_6_out, LC2);
  and and_13 (and_13_out, W4003, LC1);
  and and_14 (and_14_out, W4003, not_7_out);
  not not_7 (not_7_out, LC1);
  and and_15 (and_15_out, W4003, LC0);
  and and_16 (and_16_out, W4003, not_8_out);
  not not_8 (not_8_out, LC0);
  or or_1 (or_1_out, and_2_out, RES);
  or or_2 (or_2_out, and_4_out, RES);
  or or_3 (or_3_out, and_6_out, RES);
  or or_4 (or_4_out, and_8_out, RES);
  or or_5 (or_5_out, and_10_out, RES);
  or or_6 (or_6_out, and_12_out, RES);
  or or_7 (or_7_out, and_14_out, RES);
  or or_8 (or_8_out, and_16_out, RES);
  D_Flip_Flop d_ff_1 (
    .clk(STEP), .D(d_ff_9_qn), .Q(d_ff_1_q), .Qn(d_ff_1_qn), .preset(and_1_out), .reset(or_1_out));  // open: en
  not not_9 (not_9_out, nor_2_out);
  D_Flip_Flop d_ff_2 (
    .clk(STEP), .D(d_ff_10_qn), .Q(d_ff_2_q), .Qn(d_ff_2_qn), .preset(and_3_out), .reset(or_2_out));  // open: en
  not not_10 (not_10_out, nor_3_out);
  D_Flip_Flop d_ff_3 (
    .clk(STEP), .D(d_ff_11_qn), .Q(d_ff_3_q), .Qn(d_ff_3_qn), .preset(and_5_out), .reset(or_3_out));  // open: en
  not not_11 (not_11_out, nor_4_out);
  D_Flip_Flop d_ff_4 (
    .clk(STEP), .D(d_ff_12_qn), .Q(d_ff_4_q), .Qn(d_ff_4_qn), .preset(and_7_out), .reset(or_4_out));  // open: en
  not not_12 (not_12_out, nor_5_out);
  D_Flip_Flop d_ff_5 (
    .clk(STEP), .D(d_ff_13_qn), .Q(d_ff_5_q), .Qn(d_ff_5_qn), .preset(and_9_out), .reset(or_5_out));  // open: en
  not not_13 (not_13_out, nor_6_out);
  D_Flip_Flop d_ff_6 (
    .clk(STEP), .D(d_ff_14_qn), .Q(d_ff_6_q), .Qn(d_ff_6_qn), .preset(and_11_out), .reset(or_6_out));  // open: en
  not not_14 (not_14_out, nor_7_out);
  D_Flip_Flop d_ff_7 (
    .clk(STEP), .D(d_ff_15_qn), .Q(d_ff_7_q), .Qn(d_ff_7_qn), .preset(and_13_out), .reset(or_7_out));  // open: en
  not not_15 (not_15_out, nor_8_out);
  D_Flip_Flop d_ff_8 (
    .clk(STEP), .D(d_ff_16_qn), .Q(d_ff_8_q), .Qn(d_ff_8_qn), .preset(and_15_out), .reset(or_8_out));  // open: en
  not not_16 (not_16_out, HALT);
  D_Flip_Flop d_ff_9 (.clk(nACLK), .D(multiplexer_1_out), .Qn(d_ff_9_qn));  // open: Q, preset, en, reset
  Multiplexer multiplexer_1 (.in0(d_ff_1_qn), .in1(d_ff_1_q), .out(multiplexer_1_out), .sel(nor_2_out));  // open: en
  D_Flip_Flop d_ff_10 (.clk(nACLK), .D(multiplexer_2_out), .Qn(d_ff_10_qn));  // open: Q, preset, en, reset
  Multiplexer multiplexer_2 (.in0(d_ff_2_qn), .in1(d_ff_2_q), .out(multiplexer_2_out), .sel(nor_3_out));  // open: en
  D_Flip_Flop d_ff_11 (.clk(nACLK), .D(multiplexer_3_out), .Qn(d_ff_11_qn));  // open: Q, preset, en, reset
  Multiplexer multiplexer_3 (.in0(d_ff_3_qn), .in1(d_ff_3_q), .out(multiplexer_3_out), .sel(nor_4_out));  // open: en
  D_Flip_Flop d_ff_12 (.clk(nACLK), .D(multiplexer_4_out), .Qn(d_ff_12_qn));  // open: Q, preset, en, reset
  Multiplexer multiplexer_4 (.in0(d_ff_4_qn), .in1(d_ff_4_q), .out(multiplexer_4_out), .sel(nor_5_out));  // open: en
  D_Flip_Flop d_ff_13 (.clk(nACLK), .D(multiplexer_5_out), .Qn(d_ff_13_qn));  // open: Q, preset, en, reset
  Multiplexer multiplexer_5 (.in0(d_ff_5_qn), .in1(d_ff_5_q), .out(multiplexer_5_out), .sel(nor_6_out));  // open: en
  D_Flip_Flop d_ff_14 (.clk(nACLK), .D(multiplexer_6_out), .Qn(d_ff_14_qn));  // open: Q, preset, en, reset
  Multiplexer multiplexer_6 (.in0(d_ff_6_qn), .in1(d_ff_6_q), .out(multiplexer_6_out), .sel(nor_7_out));  // open: en
  D_Flip_Flop d_ff_15 (.clk(nACLK), .D(multiplexer_7_out), .Qn(d_ff_15_qn));  // open: Q, preset, en, reset
  Multiplexer multiplexer_7 (.in0(d_ff_7_qn), .in1(d_ff_7_q), .out(multiplexer_7_out), .sel(nor_8_out));  // open: en
  D_Flip_Flop d_ff_16 (.clk(nACLK), .D(multiplexer_8_out), .Qn(d_ff_16_qn));  // open: Q, preset, en, reset
  Multiplexer multiplexer_8 (.in0(d_ff_8_qn), .in1(d_ff_8_q), .out(multiplexer_8_out), .sel(HALT));  // open: en
  nor nor_1 (Carry_Out, d_ff_1_q, not_9_out);
  nor nor_2 (nor_2_out, d_ff_2_q, not_10_out);
  nor nor_3 (nor_3_out, d_ff_3_q, not_11_out);
  nor nor_4 (nor_4_out, d_ff_4_q, not_12_out);
  nor nor_5 (nor_5_out, d_ff_5_q, not_13_out);
  nor nor_6 (nor_6_out, d_ff_6_q, not_14_out);
  nor nor_7 (nor_7_out, d_ff_7_q, not_15_out);
  nor nor_8 (nor_8_out, d_ff_8_q, not_16_out);
endmodule
