// Logisim project APUPlayer.circ as structural Verilog: 7 circuits, main circuit AUXDumper
module APUPlayer (
  input  nRES
);

  wire apu_dmc, apu_m2__ext, apu_nirq_cpu, apu_nnmi_cpu, apu_phi0__cpu, apu_r_w__ext, apu_rdy__cpu,
       apu_rmode, apu_rnd, apu_sqa, apu_sqb, apu_tri, core_phi1, core_phi2, core_r_w, XTAL_out;
  wire [1:0] apu_sqa_duty, apu_sqb_duty;
  wire [3:0] apu_n_req, transp_latch_q_2, transp_latch_q_3;
  wire [5:0] apu_n_env, apu_sqa_env, apu_sqb_env;
  wire [7:0] apu_aux_a, apu_data_to_cpu, apu_db_out, apu_sw_a, apu_sw_b, apu_tri_lin, core_db_out,
       transp_latch_q, wram_db_out;
  wire [10:0] apu_sqa_f, apu_sqb_f, apu_tri_freq;
  wire [14:0] apu_aux_b;
  wire [15:0] apu_ab, core_addr;
  wire [23:0] dumper_addr;
  wire [31:0] dumper_data;

  Clock XTAL (.out(XTAL_out));
  LED DMC (.in(apu_dmc));
  LED TRI (.in(apu_tri));
  LED SQB (.in(apu_sqb));
  LED SQA (.in(apu_sqa));
  LED RND (.in(apu_rnd));
  LED led_1 (.in(apu_tri_freq[0]));
  LED led_2 (.in(apu_tri_freq[1]));
  LED led_3 (.in(apu_tri_freq[2]));
  LED led_4 (.in(apu_tri_freq[3]));
  LED led_5 (.in(apu_tri_freq[4]));
  LED led_6 (.in(apu_tri_freq[5]));
  LED led_7 (.in(apu_tri_freq[6]));
  LED led_8 (.in(apu_tri_freq[7]));
  LED led_9 (.in(apu_tri_freq[8]));
  LED led_10 (.in(apu_tri_freq[9]));
  LED led_11 (.in(apu_tri_freq[10]));
  LED led_12 (.in(apu_tri_lin[0]));
  LED led_13 (.in(apu_tri_lin[1]));
  LED led_14 (.in(apu_tri_lin[2]));
  LED led_15 (.in(apu_tri_lin[3]));
  LED led_16 (.in(apu_tri_lin[4]));
  LED led_17 (.in(apu_tri_lin[5]));
  LED led_18 (.in(apu_tri_lin[6]));
  LED TRI_RELOAD (.in(apu_tri_lin[7]));
  _2A03_APU apu (
    .nRES_PIN(nRES), .RDY__CPU(apu_rdy__cpu), .R_W__CPU(core_r_w), .nIRQ_CPU(apu_nirq_cpu),
    .nNMI_CPU(apu_nnmi_cpu), .nNMI_PIN(1'b1), .R_W__EXT(apu_r_w__ext), .DBG__EXT(1'b0),
    .M2__EXT(apu_m2__ext), .PHI0__CPU(apu_phi0__cpu), .nIRQ_PIN(1'b1), .Data_to_CPU(apu_data_to_cpu),
    .Data_from_CPU(core_db_out), .AUX_A(apu_aux_a), .AUX_B(apu_aux_b), .CPU_Ax(core_addr), .AB(apu_ab),
    .DB_in(wram_db_out), .DB_out(apu_db_out), .PHI1_FromCore(core_phi1), .PHI2_FromCore(core_phi2),
    .CLK(XTAL_out), .RND(apu_rnd), .TRI(apu_tri), .SQB(apu_sqb), .SQA(apu_sqa), .DMC(apu_dmc),
    .SQA_F(apu_sqa_f), .SW_B(apu_sw_b), .SW_A(apu_sw_a), .SQB_F(apu_sqb_f), .N_ENV(apu_n_env),
    .RMODE(apu_rmode), .N_REQ(apu_n_req), .SQB_ENV(apu_sqb_env), .SQB_DUTY(apu_sqb_duty),
    .SQA_DUTY(apu_sqa_duty), .SQA_ENV(apu_sqa_env), .TRI_LIN(apu_tri_lin), .TRI_FREQ(apu_tri_freq));  // open: OUT0, OUT1, OUT2, nIN0, nIN1
  LED led_19 (.in(apu_sqa_f[0]));
  LED led_20 (.in(apu_sqa_f[1]));
  LED led_21 (.in(apu_sqa_f[2]));
  LED led_22 (.in(apu_sqa_f[3]));
  LED led_23 (.in(apu_sqa_f[4]));
  LED led_24 (.in(apu_sqa_f[5]));
  LED led_25 (.in(apu_sqa_f[6]));
  LED led_26 (.in(apu_sqa_f[7]));
  LED led_27 (.in(apu_sqa_f[8]));
  LED led_28 (.in(apu_sqa_f[9]));
  LED led_29 (.in(apu_sqa_f[10]));
  LED SQA_ENV (.in(apu_sqa_env[0]));
  LED led_30 (.in(apu_sqa_env[1]));
  LED led_31 (.in(apu_sqa_env[2]));
  LED led_32 (.in(apu_sqa_env[3]));
  LED ENVDIS (.in(apu_sqa_env[4]));
  LED HALT_SQA (.in(apu_sqa_env[5]));
  LED SQA_DUTY (.in(apu_sqa_duty[0]));
  LED led_33 (.in(apu_sqa_duty[1]));
  LED led_34 (.in(apu_sw_a[0]));
  LED led_35 (.in(apu_sw_a[1]));
  LED led_36 (.in(apu_sw_a[2]));
  LED led_37 (.in(apu_sw_a[3]));
  LED led_38 (.in(apu_sw_a[4]));
  LED led_39 (.in(apu_sw_a[5]));
  LED led_40 (.in(apu_sw_a[6]));
  LED led_41 (.in(apu_sw_a[7]));
  LED led_42 (.in(apu_sqb_f[0]));
  LED led_43 (.in(apu_sqb_f[1]));
  LED led_44 (.in(apu_sqb_f[2]));
  LED led_45 (.in(apu_sqb_f[3]));
  LED led_46 (.in(apu_sqb_f[4]));
  LED led_47 (.in(apu_sqb_f[5]));
  LED led_48 (.in(apu_sqb_f[6]));
  LED led_49 (.in(apu_sqb_f[7]));
  LED led_50 (.in(apu_sqb_f[8]));
  LED led_51 (.in(apu_sqb_f[9]));
  LED led_52 (.in(apu_sqb_f[10]));
  LED SQB_ENV (.in(apu_sqb_env[0]));
  LED led_53 (.in(apu_sqb_env[1]));
  LED led_54 (.in(apu_sqb_env[2]));
  LED led_55 (.in(apu_sqb_env[3]));
  LED ENVDIS_2 (.in(apu_sqb_env[4]));
  LED HALT_SQB (.in(apu_sqb_env[5]));
  WRAM wram (
    .M2(apu_m2__ext), .Addr(apu_ab), .DB_in(apu_db_out), .R_W(apu_r_w__ext), .nRES(nRES), .DB_out(wram_db_out));
  Fake6502 core (
    .PHI0(apu_phi0__cpu), .RDY(apu_rdy__cpu), .SO(1'b1), .nNMI(apu_nnmi_cpu), .nIRQ(apu_nirq_cpu),
    .nRES(nRES), .DB_in(apu_data_to_cpu), .PHI1(core_phi1), .PHI2(core_phi2), .R_W(core_r_w),
    .Addr(core_addr), .DB_out(core_db_out));  // open: SYNC
  LED SQB_DUTY (.in(apu_sqb_duty[0]));
  LED led_56 (.in(apu_sqb_duty[1]));
  LED led_57 (.in(apu_sw_b[0]));
  LED led_58 (.in(apu_sw_b[1]));
  LED led_59 (.in(apu_sw_b[2]));
  LED led_60 (.in(apu_sw_b[3]));
  LED led_61 (.in(apu_sw_b[4]));
  LED led_62 (.in(apu_sw_b[5]));
  LED led_63 (.in(apu_sw_b[6]));
  LED led_64 (.in(apu_sw_b[7]));
  LED RMODE (.in(apu_rmode));
  LED NFREQ (.in(apu_n_req[0]));
  LED led_65 (.in(apu_n_req[1]));
  LED led_66 (.in(apu_n_req[2]));
  LED led_67 (.in(apu_n_req[3]));
  LED N_ENV (.in(apu_n_env[0]));
  LED led_68 (.in(apu_n_env[1]));
  LED led_69 (.in(apu_n_env[2]));
  LED led_70 (.in(apu_n_env[3]));
  LED ENVDIS_3 (.in(apu_n_env[4]));
  LED HALT_NOISE (.in(apu_n_env[5]));
  AUXDumper dumper (.PHI1(core_phi1), .AUX({1'b0, apu_aux_b, apu_aux_a}), .Addr(dumper_addr), .Data(dumper_data));
  Hex_Digit_Display hex_digit_display_1 (.value(transp_latch_q_3));  // open: dp
  Register #(.width(16), .trigger("high")) transp_latch (
    .D(core_addr), .en(core_addr[14]), .Q({transp_latch_q_3, transp_latch_q_2, transp_latch_q}),
    .clk(core_phi2));  // open: clr
  Hex_Digit_Display hex_digit_display_2 (.value(transp_latch_q[7:4]));  // open: dp
  Hex_Digit_Display hex_digit_display_3 (.value(transp_latch_q_2));  // open: dp
  Hex_Digit_Display hex_digit_display_4 (.value(transp_latch_q[3:0]));  // open: dp
  RAM #(.addrWidth(24), .dataWidth(32), .bus("asynch")) ram_1 (
    .addr(dumper_addr), .data(dumper_data), .sel(1'b1), .ld(1'b0), .clr(1'b0));

  // Notes on the sheet:
  //   TRI_F
  //   TRI_LIN
  //   SQA_F
  //   SW_A
  //   N.C.
  //   SQB_F
  //   SW_B
  //   Load regdump here
  //   Last APU Register
  //   Taram-param-pam. Pam! Peep, peep, peep. Pipipipip, pip, pibibip
endmodule

module AUXDumper (
  input  PHI1,
  input  [23:0] AUX,
  output [23:0] Addr,
  output [31:0] Data
);

  wire adder_1_p3, counter_2_q, counter_3_q;
  wire [31:0] aux_a_1_a, aux_b_1_a;

  AUX_A aux_a_1 (.d(AUX[7:0]), .a(aux_a_1_a));
  AUX_B aux_b_1 (.d(AUX[23:8]), .a(aux_b_1_a));
  Counter #(.width(23), .max('h7fffff)) counter_1 (.Q(Addr[23:1]), .clk(PHI1));  // open: load, D, count, carry, clr
  Counter #(.width(1), .max('h1)) counter_2 (.Q(counter_2_q), .clk(PHI1));  // open: load, D, count, carry, clr
  Counter #(.width(1), .max('h1), .trigger("falling")) counter_3 (
    .Q(counter_3_q), .clk(PHI1));  // open: load, D, count, carry, clr
  // Adder adder_1: pin names not known; wires that end beside it: aux_a_1_a, aux_b_1_a, adder_1_p3
  // Divider divider_1: pin names not known; wires that end beside it: adder_1_p3, 32'h40000000, Data
  xnor xnor_1 (Addr[0], counter_2_q, counter_3_q);

  // Notes on the sheet:
  //   a + b
  //   The invention of the org to make the ADDR tick EVERY half cycle.
  //    : 2
  //   normalized samples in range [0.0f; 1.0f]
endmodule

module AUX_A (
  input  [7:0] d,
  output [31:0] a
);

  ROM #(.dataWidth(32)) rom_1 (.addr(d), .data(a), .sel(1'b1));

  // Notes on the sheet:
  //   0...255
  //   contents of rom_1 (hex, n*v repeats v):
  //   3ab77b8e 3d12a8ec 3d924925 3ddadec7 3e118b0c 3e3577e6 3e59364e 3e7cc69c 3e901495 3ea1af28 3eb33333
  //   3ec4a0e1 3ed5f85c 3ee739ce 3ef86563 3f04bda1 3d12a8ec 3d924925 3ddadec7 3e118b0c 3e3577e6 3e59364e
  //   3e7cc69c 3e901495 3ea1af28 3eb33333 3ec4a0e1 3ed5f85c 3ee739ce 3ef86563 3f04bda1 3f0d3dcb 3d924925
  //   3ddadec7 3e118b0c 3e3577e6 3e59364e 3e7cc69c 3e901495 3ea1af28 3eb33333 3ec4a0e1 3ed5f85c 3ee739ce
  //   3ef86563 3f04bda1 3f0d3dcb 3f15b343 3ddadec7 3e118b0c 3e3577e6 3e59364e 3e7cc69c 3e901495 3ea1af28
  //   3eb33333 3ec4a0e1 3ed5f85c 3ee739ce 3ef86563 3f04bda1 3f0d3dcb 3f15b343 3f1e1e1e 3e118b0c 3e3577e6
  //   3e59364e 3e7cc69c 3e901495 3ea1af28 3eb33333 3ec4a0e1 3ed5f85c 3ee739ce 3ef86563 3f04bda1 3f0d3dcb
  //   3f15b343 3f1e1e1e 3f267e6f 3e3577e6 3e59364e 3e7cc69c 3e901495 3ea1af28 3eb33333 3ec4a0e1 3ed5f85c
  //   3ee739ce 3ef86563 3f04bda1 3f0d3dcb 3f15b343 3f1e1e1e 3f267e6f 3f2ed44b 3e59364e 3e7cc69c 3e901495
  //   3ea1af28 3eb33333 3ec4a0e1 3ed5f85c 3ee739ce 3ef86563 3f04bda1 3f0d3dcb 3f15b343 3f1e1e1e 3f267e6f
  //   3f2ed44b 3f371fc4 3e7cc69c 3e901495 3ea1af28 3eb33333 3ec4a0e1 3ed5f85c 3ee739ce 3ef86563 3f04bda1
  //   3f0d3dcb 3f15b343 3f1e1e1e 3f267e6f 3f2ed44b 3f371fc4 3f3f60ef 3e901495 3ea1af28 3eb33333 3ec4a0e1
  //   3ed5f85c 3ee739ce 3ef86563 3f04bda1 3f0d3dcb 3f15b343 3f1e1e1e 3f267e6f 3f2ed44b 3f371fc4 3f3f60ef
  //   3f4797dd 3ea1af28 3eb33333 3ec4a0e1 3ed5f85c 3ee739ce 3ef86563 3f04bda1 3f0d3dcb 3f15b343 3f1e1e1e
  //   3f267e6f 3f2ed44b 3f371fc4 3f3f60ef 3f4797dd 3f4fc4a3 3eb33333 3ec4a0e1 3ed5f85c 3ee739ce 3ef86563
  //   3f04bda1 3f0d3dcb 3f15b343 3f1e1e1e 3f267e6f 3f2ed44b 3f371fc4 3f3f60ef 3f4797dd 3f4fc4a3 3f57e753
  //   3ec4a0e1 3ed5f85c 3ee739ce 3ef86563 3f04bda1 3f0d3dcb 3f15b343 3f1e1e1e 3f267e6f 3f2ed44b 3f371fc4
  //   3f3f60ef 3f4797dd 3f4fc4a3 3f57e753 3f600000 3ed5f85c 3ee739ce 3ef86563 3f04bda1 3f0d3dcb 3f15b343
  //   3f1e1e1e 3f267e6f 3f2ed44b 3f371fc4 3f3f60ef 3f4797dd 3f4fc4a3 3f57e753 3f600000 3f680ebc 3ee739ce
  //   3ef86563 3f04bda1 3f0d3dcb 3f15b343 3f1e1e1e 3f267e6f 3f2ed44b 3f371fc4 3f3f60ef 3f4797dd 3f4fc4a3
  //   3f57e753 3f600000 3f680ebc 3f701399 3ef86563 3f04bda1 3f0d3dcb 3f15b343 3f1e1e1e 3f267e6f 3f2ed44b
  //   3f371fc4 3f3f60ef 3f4797dd 3f4fc4a3 3f57e753 3f600000 3f680ebc 3f701399 3f780eaa 3f04bda1 3f0d3dcb
  //   3f15b343 3f1e1e1e 3f267e6f 3f2ed44b 3f371fc4 3f3f60ef 3f4797dd 3f4fc4a3 3f57e753 3f600000 3f680ebc
  //   3f701399 3f780eaa 3f800000
endmodule

module AUX_B (
  input  [15:0] d,
  output [31:0] a
);

  ROM #(.addrWidth(15), .dataWidth(32)) rom_1 (.addr(d[14:0]), .data(a), .sel(1'b1));

  // Notes on the sheet:
  //   0...32767
  //   contents of rom_1 (hex, n*v repeats v):
  //   39f0dbd4 3cc007b4 3d3f0e2a 3d8e915b 3dbd229a 3deb3ca3 3e0c709f 3e230913 3e39688b 3e4f8fdb 3e657fd7
  //   3e7b394d 3e885e84 3e9305e6 3e9d932f 3ea806be 3c40856f 3d0fa7f6 3d6e36ed 3da5e8fe 3dd43e69 3e010ec1
  //   3e17c406 3e2e3fe1 3e44832b 3e5a8eb7 3e706356 3e8300eb 3e8db57e 3e984fc8 3ea2d028 3ead36fd 3cc007b4
  //   3d3f0e2a 3d8e915b 3dbd229a 3deb3ca3 3e0c709f 3e230913 3e39688b 3e4f8fdb 3e657fd7 3e7b394d 3e885e84
  //   3e9305e6 3e9d932f 3ea806be 3eb260f0 3d0fa7f6 3d6e36ed 3da5e8fe 3dd43e69 3e010ec1 3e17c406 3e2e3fe1
  //   3e44832b 3e5a8eb7 3e706356 3e8300eb 3e8db57e 3e984fc8 3ea2d028 3ead36fd 3eb784a4 3d3f0e2a 3d8e915b
  //   3dbd229a 3deb3ca3 3e0c709f 3e230913 3e39688b 3e4f8fdb 3e657fd7 3e7b394d 3e885e84 3e9305e6 3e9d932f
  //   3ea806be 3eb260f0 3ebca222 3d6e36ed 3da5e8fe 3dd43e69 3e010ec1 3e17c406 3e2e3fe1 3e44832b 3e5a8eb7
  //   3e706356 3e8300eb 3e8db57e 3e984fc8 3ea2d028 3ead36fd 3eb784a4 3ec1b977 3d8e915b 3dbd229a 3deb3ca3
  //   3e0c709f 3e230913 3e39688b 3e4f8fdb 3e657fd7 3e7b394d 3e885e84 3e9305e6 3e9d932f 3ea806be 3eb260f0
  //   3ebca222 3ec6caae 3da5e8fe 3dd43e69 3e010ec1 3e17c406 3e2e3fe1 3e44832b 3e5a8eb7 3e706356 3e8300eb
  //   3e8db57e 3e984fc8 3ea2d028 3ead36fd 3eb784a4 3ec1b977 3ecbd5d1 3dbd229a 3deb3ca3 3e0c709f 3e230913
  //   3e39688b 3e4f8fdb 3e657fd7 3e7b394d 3e885e84 3e9305e6 3e9d932f 3ea806be 3eb260f0 3ebca222 3ec6caae
  //   3ed0daec 3dd43e69 3e010ec1 3e17c406 3e2e3fe1 3e44832b 3e5a8eb7 3e706356 3e8300eb 3e8db57e 3e984fc8
  //   3ea2d028 3ead36fd 3eb784a4 3ec1b977 3ecbd5d1 3ed5da09 3deb3ca3 3e0c709f 3e230913 3e39688b 3e4f8fdb
  //   3e657fd7 3e7b394d 3e885e84 3e9305e6 3e9d932f 3ea806be 3eb260f0 3ebca222 3ec6caae 3ed0daec 3edad333
  //   3e010ec1 3e17c406 3e2e3fe1 3e44832b 3e5a8eb7 3e706356 3e8300eb 3e8db57e 3e984fc8 3ea2d028 3ead36fd
  //   3eb784a4 3ec1b977 3ecbd5d1 3ed5da09 3edfc674 3e0c709f 3e230913 3e39688b 3e4f8fdb 3e657fd7 3e7b394d
  //   3e885e84 3e9305e6 3e9d932f 3ea806be 3eb260f0 3ebca222 3ec6caae 3ed0daec 3edad333 3ee4b3d8 3e17c406
  //   3e2e3fe1 3e44832b 3e5a8eb7 3e706356 3e8300eb 3e8db57e 3e984fc8 3ea2d028 3ead36fd 3eb784a4 3ec1b977
  //   3ecbd5d1 3ed5da09 3edfc674 3ee99b68 3e230913 3e39688b 3e4f8fdb 3e657fd7 3e7b394d 3e885e84 3e9305e6
  //   3e9d932f 3ea806be 3eb260f0 3ebca222 3ec6caae 3ed0daec 3edad333 3ee4b3d8 3eee7d2e 3e2e3fe1 3e44832b
  //   3e5a8eb7 3e706356 3e8300eb 3e8db57e 3e984fc8 3ea2d028 3ead36fd 3eb784a4 3ec1b977 3ecbd5d1 3ed5da09
  //   3edfc674 3ee99b68 3ef35936 3bc0c48a 3cefbb5a 3d56aa32 3d9a40f1 3dc8b438 3df6b0bb 3e121c1f 3e28a641
  //   3e3ef79a 3e551102 3e6af34a 3e804f9f 3e8b0ad4 3e95aba7 3ea03278 3eaa9fa7 3c9034de 3d2762c6 3d82da35
  //   3db1898a 3ddfc135 3e06c180 3e1d6856 3e33d5f9 3e4a0b3f 3e6008fd 3e75d001 3e85b08c 3e905e84 3e9af24a
  //   3ea56c3e 3eafccbf 3cefbb5a 3d56aa32 3d9a40f1 3dc8b438 3df6b0bb 3e121c1f 3e28a641 3e3ef79a 3e551102
  //   3e6af34a 3e804f9f 3e8b0ad4 3e95aba7 3ea03278 3eaa9fa7 3eb4f391 3d2762c6 3d82da35 3db1898a 3ddfc135
  //   3e06c180 3e1d6856 3e33d5f9 3e4a0b3f 3e6008fd 3e75d001 3e85b08c 3e905e84 3e9af24a 3ea56c3e 3eafccbf
  //   3eba1429 3d56aa32 3d9a40f1 3dc8b438 3df6b0bb 3e121c1f 3e28a641 3e3ef79a 3e551102 3e6af34a 3e804f9f
  //   3e8b0ad4 3e95aba7 3ea03278 3eaa9fa7 3eb4f391 3ebf2e91 3d82da35 3db1898a 3ddfc135 3e06c180 3e1d6856
  //   3e33d5f9 3e4a0b3f 3e6008fd 3e75d001 3e85b08c 3e905e84 3e9af24a 3ea56c3e 3eafccbf 3eba1429 3ec442d6
  //   3d9a40f1 3dc8b438 3df6b0bb 3e121c1f 3e28a641 3e3ef79a 3e551102 3e6af34a 3e804f9f 3e8b0ad4 3e95aba7
  //   3ea03278 3eaa9fa7 3eb4f391 3ebf2e91 3ec95101 3db1898a 3ddfc135 3e06c180 3e1d6856 3e33d5f9 3e4a0b3f
  //   3e6008fd 3e75d001 3e85b08c 3e905e84 3e9af24a 3ea56c3e 3eafccbf 3eba1429 3ec442d6 3ece591f 3dc8b438
  //   3df6b0bb 3e121c1f 3e28a641 3e3ef79a 3e551102 3e6af34a 3e804f9f 3e8b0ad4 3e95aba7 3ea03278 3eaa9fa7
  //   3eb4f391 3ebf2e91 3ec95101 3ed35b39 3ddfc135 3e06c180 3e1d6856 3e33d5f9 3e4a0b3f 3e6008fd 3e75d001
  //   3e85b08c 3e905e84 3e9af24a 3ea56c3e 3eafccbf 3eba1429 3ec442d6 3ece591f 3ed8575b 3df6b0bb 3e121c1f
  //   3e28a641 3e3ef79a 3e551102 3e6af34a 3e804f9f 3e8b0ad4 3e95aba7 3ea03278 3eaa9fa7 3eb4f391 3ebf2e91
  //   3ec95101 3ed35b39 3edd4d90 3e06c180 3e1d6856 3e33d5f9 3e4a0b3f 3e6008fd 3e75d001 3e85b08c 3e905e84
  //   3e9af24a 3ea56c3e 3eafccbf 3eba1429 3ec4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
endmodule

module Fake6502 (
  input  PHI0,
  input  RDY,
  input  SO,
  input  nNMI,
  input  nIRQ,
  input  nRES,
  input  [7:0] DB_in,
  output PHI1,
  output PHI2,
  output R_W,
  output SYNC,
  output [15:0] Addr,
  output [7:0] DB_out
);

  wire [23:0] redump_redump_addr;
  wire [31:0] rom_1_data;

  ROM #(.addrWidth(24), .dataWidth(32)) rom_1 (.addr(redump_redump_addr), .data(rom_1_data), .sel(1'b1));
  RegDumpProcessor redump (
    .PHI0(PHI0), .regdump_data(rom_1_data), .Core_R_W(R_W), .Core_AB(Addr), .Core_DB(DB_out),
    .redump_addr(redump_redump_addr));
  not not_1 (PHI1, PHI0);

  assign PHI2 = PHI0;
  assign SYNC = 1'b0;

  // Notes on the sheet:
  //   N.C.
  //   N.C.
  //   N.C.
  //   Load regdump here
  //   contents of rom_1 (hex, n*v repeats v):
  //   ec b15 6 f15 67 a906 b 807 3b 8204 4 7f05 4b 9004 6 7f05 69 2e02 b 903 3b 7f01 4 8200 43 9000 c 7f01
  //   44 1f08 28 7c0a b 90b 85 1c0c 4 30e 4 580f 36 11 12 116 8 16 6d94 214 331 ff17 6 f15 c1 9804 6 7f05
  //   4b 9800 c 7f01 52 111 12 116 8 16 6f94 214 320 ff17 6 f15 c1 9704 6 7f05 4b 9700 c 7f01 52 211 12
  //   116 8 16 6fa5 214 26e ff17 6 f15 c1 9604 6 7f05 4b 9600 c 7f01 52 311 12 116 8 16 7058 214 26e ff17
  //   6 f15 c1 9504 6 7f05 4b 9500 c 7f01 52 411 12 116 8 16 7054 214 331 ff17 6 f15 c1 9504 6 7f05 4b
  //   9500 c 7f01 52 511 12 116 8 16 6f95 214 26e ff17 6 f15 c1 9404 6 7f05 4b 9400 c 7f01 52 611 12 116 8
  //   16 7056 214 26e ff17 6 f15 c1 9404 6 7f05 4b 9400 c 7f01 52 711 12 116 8 16 7058 214 26e ff17 6 f15
  //   bc 9004 6 7f05 46 9000 c 7f01 52 811 12 116 8 16 705e 214 26e ff17 6 f15 e2 a906 b 807 3b 8204 4
  //   7f05 4b 9004 6 7f05 69 2e02 b 903 3b 7f01 4 8200 43 9000 c 7f01 44 1f08 28 7c0a b 90b 64 911 12 116
  //   8 16 6e6f 214 26f ff17 6 f15 c1 9804 6 7f05 4b 9800 c 7f01 52 a11 12 116 8 16 7055 214 26f ff17 6
  //   f15 c1 9704 6 7f05 4b 9700 c 7f01 52 b11 12 116 8 16 7056 214 26e ff17 6 f15 c1 9604 6 7f05 4b 9600
  //   c 7f01 52 c11 12 116 8 16 7056 214 331 ff17 6 f15 c1 9504 6 7f05 4b 9500 c 7f01 52 d11 12 116 8 16
  //   6f94 214 26f ff17 6 f15 c1 9504 6 7f05 4b 9500 c 7f01 52 e11 12 116 8 16 7053 214 26f ff17 6 f15 c1
  //   9404 6 7f05 4b 9400 c 7f01 52 f11 12 116 8 16 7056 214 26e ff17 6 f15 c1 9404 6 7f05 4b 9400 c 7f01
  //   52 1011 12 116 8 16 7056 214 26e ff17 6 f15 bc 9004 6 7f05 46 9000 c 7f01 52 1111 12 116 8 16 7063
  //   214 26f ff17 6 f15 bc 9004 6 7f05 46 9000 c 7f01 7a 1c0c 4 30e 4 180f 36 1211 12 116 8 16 6ff7 214
  //   26f ff17 6 f15 bc 9004 6 7f05 46 9000 c 7f01 52 1311 12 116 8 16 7061 214 26f ff17 6 f15 bc 9004 6
  //   7f05 46 9000 c 7f01 52 1411 12 116 8 16 7060 214 331 ff17 6 f15 bc 9004 6 7f05 46 9000 c 7f01 52
  //   1511 12 116 8 16 6f9d 214 26e ff17 6 f15 bc 9004 6 7f05 46 9000 c 7f01 52 1611 12 116 8 16 7060 214
  //   26e ff17 6 f15 bc 9004 6 7f05 46 9000 c 7f01 52 1711 12 116 8 16 7061 214 26f ff17 6 f15 bc 9004 6
  //   7f05 46 9000 c 7f01 52 1811 12 116 8 16 705f 214 26f ff17 6 f15 bc 9004 6 7f05 46 9000 c 7f01 52
  //   1911 12 116 8 16 7060 214 31f ff17 6 f15 bc 9004 6 7f05 46 9000 c 7f01 52 1a11 12 116 8 16 6faf 214
  //   26e ff17 6 f15 b2 a906 b 807 3b 8204 4 7f05 4b 9004 6 7f05 69 2e02 b 903 3b 7f01 4 8200 43 9000 c
  //   7f01 36 7c0a b 90b 85 1c0c 4 30e 4 580f 36 1b11 12 116 8 16 6e75 214 26e ff17 6 f15 c1 9804 6 7f05
  //   4b 9800 c 7f01 52 1c11 12 116 8 16 7056 214 331 ff17 6 f15 c1 9704 6 7f05 4b 9700 c 7f01 52 1d11 12
  //   116 8 16 6f92 214 26f ff17 6 f15 c1 9604 6 7f05 4b 9600 c 7f01 52 1e11 12 116 8 16 7057 214 26f ff17
  //   6 f15 c1 9504 6 7f05 4b 9500 c 7f01 52 1f11 12 116 8 16 7054 214 26e ff17 6 f15 c1 9504 6 7f05 4b
  //   9500 c 7f01 52 2011 12 116 8 16 7056 214 26e ff17 6 f15 c1 9404 6 7f05 4b 9400 c 7f01 52 2111 12 116
  //   8 16 7058 214 26e ff17 6 f15 c1 9404 6 7f05 4b 9400 c 7f01 52 2211 12 116 8 16 7056 214 26e ff17 6
  //   f15 bc 9004 6 7f05 46 9000 c 7f01 52 2311 12 116 8 16 7062 214 26e ff17 6 f15 bc 9004 6 7f05 46 9000
  //   c 7f01 52 2411 12 116 8 16 7060 214 331 ff17 6 f15 bc 9004 6 7f05 46 9000 c 7f01 52 2511 12 116 8 16
  //   6f9c 214 26f ff17 6 f15 bc 9004 6 7f05 46 9000 c 7f01 52 2611 12 116 8 16 7060 214 26e ff17 6 f15 bc
  //   9004 6 7f05 46 9000 c 7f01 52 2711 12 116 8 16 7061 214 26f ff17 6 f15 bc 9004 6 7f05 46 9000 c 7f01
  //   52 2811 12 116 8 16 705f 214 26f ff17 6 f15 bc 9004 6 7f05 46 9000 c 7f01 52 2911 12 116 8 16 7060
  //   214 26e ff17 6 f15 bc 9004 6 7f05 46 9000 c 7f01 52 2a11 12 116 8 16 7061 214 26f ff17 6 f15 bc 9004
  //   6 7f05 46 9000 c 7f01 52 2b11 12 116 8 16 705e 214 26e ff17 6 f15 bc 9004 6 7f05 46 9000 c 7f01 52
  //   2c11 12 116 8 16 7060 214 331 ff17 6 f15 e2 d506 b 807 3b 8204 4 7f05 4b 9004 6 7f05 69 2e02 b 903
  //   3b 7f01 4 8200 43 9000 c 7f01 44 1f08 28 7c0a b 90b 8c 1c0c 4 30e 4 180f 36 2d11 12 116 8 16 6d45
  //   214 26e ff17 6 f15 c1 9804 6 7f05 4b 9800 c 7f01 52 2e11 12 116 8 16 7057 214 26f ff17 6 f15 c1 9704
  //   6 7f05 4b 9700 c 7f01 52 2f11 12 116 8 16 7055 214 26f ff17 6 f15 c1 9604 6 7f05 4b 9600 c 7f01 5b
  //   3011 12 116 8 16 704d 2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
endmodule

module WRAM (
  input  M2,
  input  [15:0] Addr,
  input  [7:0] DB_in,
  input  R_W,
  input  nRES,
  output [7:0] DB_out
);

  wire nor_1_out, not_1_out, not_2_out;

  not not_1 (not_1_out, nRES);
  nor nor_1 (nor_1_out, Addr[11], Addr[12], Addr[13], Addr[14], Addr[15]);
  not not_2 (not_2_out, R_W);
  RAM #(.addrWidth(11), .bus("separate")) ram_1 (
    .addr(Addr[10:0]), .din(DB_in), .data(DB_out), .str(not_2_out), .sel(nor_1_out), .clk(M2), .ld(R_W),
    .clr(not_1_out));
endmodule

module RegDumpProcessor (
  input  PHI0,
  input  [31:0] regdump_data,
  output Core_R_W,
  output [15:0] Core_AB,
  output [7:0] Core_DB,
  output [23:0] redump_addr
);

  wire and_1_out, and_2_out, cnt_ovf_reg_q, comparator_1_eq, comparator_2_gt, multiplexer_1_out,
       multiplexer_2_out, not_1_out, or_1_out;
  wire [7:0] regop_word_q_2, undriven;
  wire [15:0] or_2_out;
  wire [31:0] delta_pclk_word_q, phi_dec_cnt_q, regop_word_q;

  Multiplexer #(.enable("false")) multiplexer_1 (.in0(1'b1), .in1(1'b1), .out(multiplexer_1_out), .sel(cnt_ovf_reg_q));
  Multiplexer #(.enable("false")) multiplexer_2 (.in0(1'b1), .in1(1'b0), .out(multiplexer_2_out), .sel(cnt_ovf_reg_q));
  Register #(.width(32)) delta_pclk_word (
    .D(regdump_data), .Q(delta_pclk_word_q), .clk(cnt_ovf_reg_q));  // open: en, clr
  Counter #(.width(32), .max('hffffffff), .ongoal("stay")) phi_dec_cnt (
    .load(multiplexer_1_out), .D(delta_pclk_word_q), .count(multiplexer_2_out), .Q(phi_dec_cnt_q), .clk(PHI0));  // open: carry, clr
  Register #(.width(32)) regop_word (
    .D(regdump_data), .Q({regop_word_q[31:16], regop_word_q_2, regop_word_q[7:0]}), .clk(and_1_out));  // open: en, clr
  Comparator #(.width(32)) comparator_1 (.a(phi_dec_cnt_q), .b({32{1'b0}}), .eq(comparator_1_eq));  // open: gt, lt
  Comparator #(.width(32)) comparator_2 (.a(delta_pclk_word_q), .b({32{1'b0}}), .gt(comparator_2_gt));  // open: eq, lt
  Register #(.width(1)) cnt_ovf_reg (.D(comparator_1_eq), .Q(cnt_ovf_reg_q), .clk(PHI0));  // open: en, clr
  and and_1 (and_1_out, PHI0, comparator_2_gt, comparator_1_eq, ~cnt_ovf_reg_q);  // AND_Gate
  or or_1 (or_1_out, and_1_out, cnt_ovf_reg_q);
  assign or_2_out = 16'h4000 | {{11{1'b0}}, regop_word_q[4:0]};  // OR_Gate or_2, 16 bits wide
  not not_1 (not_1_out, regop_word_q[7]);
  Multiplexer #(.enable("false")) multiplexer_3 (.in0(1'b1), .in1(regop_word_q[7]), .out(Core_R_W), .sel(and_1_out));
  Multiplexer #(.width(16), .enable("false")) multiplexer_4 (
    .in0({16{1'b0}}), .in1(or_2_out), .out(Core_AB), .sel(and_1_out));
  Multiplexer #(.width(8), .enable("false")) multiplexer_5 (
    .in0(undriven), .in1(regop_word_q_2), .out(Core_DB), .sel(and_2_out));
  and and_2 (and_2_out, and_1_out, not_1_out);
  Counter #(.width(24), .max('hffffff), .ongoal("stay"), .trigger("falling")) addr_cnt (
    .load(1'b0), .count(1'b1), .Q(redump_addr), .clk(or_1_out));  // open: D, carry, clr

  // Notes on the sheet:
  //   https://github.com/emu-russia/breaknes/blob/main/BreaksAPU/NSFPlayerInterop/RegDumpProcessor.cpp
  //   Load/Decrement Setup (1: Load; 0: Decrement)
  //   Do RegOp
  //   Load PHI Counter
  //   RegOp Setup
  //   Reg Index (0-0x1f)
  //   Reg Address
  //   Value (if write)
  //   1: Read register
  //   Default: Read address 0x0000
  //   1: RegOp + Write
  //   Falling edge
endmodule
