// Logisim project NSFPlayer.circ as structural Verilog: 3 circuits, main circuit NSFPlayer
module NSFPlayer (
  input  nRES,
  input  nIRQ,
  input  nNMI
);

  wire apu_p2, apu_p3, apu_p8, apu_p12, apu_p13, apu_p14, apu_p15, apu_p17, apu_p20, XTAL_out;
  wire [7:0] apu_p9, apu_p10, apu_p18, apu_p19, apu_p21;
  wire [14:0] apu_p22;
  wire [15:0] apu_p7, apu_p16;
  wire [23:0] dumper_addr;
  wire [31:0] dumper_data;

  Clock XTAL (.out(XTAL_out));
  // _2A03_APU apu: pin names not known; wires that end beside it: XTAL_out, apu_p2, apu_p3, nRES, nIRQ, nNMI, apu_p7, apu_p8, apu_p9, apu_p10, 1'b0, apu_p12, apu_p13, apu_p14, apu_p15, apu_p16, apu_p17, apu_p18, apu_p19, apu_p20, apu_p21, apu_p22
  BankedSRAM bank_switcher (.M2(apu_p12), .Addr(apu_p16), .Data_in(apu_p19), .R_W(apu_p17), .Data_out(apu_p10));
  // MOS_6502 core: pin names not known; wires that end beside it: apu_p13, apu_p20, 1'b1, apu_p14, apu_p15, nRES, apu_p18[0], apu_p18[1], apu_p18[2], apu_p18[3], apu_p18[4], apu_p18[5], apu_p18[6], apu_p18[7], apu_p2, apu_p3, apu_p8, apu_p7[0], apu_p7[1], apu_p7[2], apu_p7[3], apu_p7[4], apu_p7[5], apu_p7[6], apu_p7[7], apu_p7[8], apu_p7[9], apu_p7[10], apu_p7[11], apu_p7[12], apu_p7[13], apu_p7[14], apu_p7[15], apu_p9[0], apu_p9[1], apu_p9[2], apu_p9[3], apu_p9[4], apu_p9[5], apu_p9[6], apu_p9[7]
  AUXDumper dumper (.PHI1(apu_p2), .AUX({1'b0, apu_p22, apu_p21}), .Addr(dumper_addr), .Data(dumper_data));
  RAM #(.addrWidth(24), .dataWidth(32), .bus("asynch")) ram_1 (
    .addr(dumper_addr), .data(dumper_data), .sel(1'b1), .ld(1'b0), .clr(1'b0));

  // Notes on the sheet:
  //   N.C.
  //   <-- Load .nsf here
  //   Taram-param-pam. Pam! Peep, peep, peep. Pipipipip, pip, pibibip
endmodule

module AUXDumper (
  input  PHI1,
  input  [23:0] AUX,
  output [23:0] Addr,
  output [31:0] Data
);
endmodule

module BankedSRAM (
  input  M2,
  input  [15:0] Addr,
  input  [7:0] Data_in,
  input  R_W,
  output [7:0] Data_out
);
endmodule
