// Logisim project Famicom_Evo.circ as structural Verilog: 13 circuits, main circuit Famicom
module Famicom (
);

  P4 Player_1 ();  // open: OUT_0, S4016_CUP, S4016_D0
  P5 Player_2 ();  // open: OUT_0, S4017_CUP, S4017_D0, MIC
  P2 fds_port ();  // open: S4017_CUP, OUT_2, OUT_1, OUT_0, S4016_CUP, SOUND, n_IRQ, S4017_D4, S4017_D3, S4017_D2, S4017_D1, S4017_D0, S4016_D1
  U_40H368 U7_TriStateArray ();  // open: n_G1, n_G2, A1, A2, A3, A4, A5, A6, Y1, Y2, Y3, Y4, Y5, Y6
  U_40H368 U8_TriStateArray ();  // open: n_G1, n_G2, A1, A2, A3, A4, A5, A6, Y1, Y2, Y3, Y4, Y5, Y6
  APU cpu_inst ();  // open: CLK, D_In, n_IN0, n_IN1, n_NMI, n_RST, n_IRQ, D_Out, OUT_0, OUT_1, OUT_2, AUX_A, AUX_B, M2, A_Out, RnW
  P1 cartridge_port ();  // open: A_In, M2, PA_In, n_PA13, D_In, PD_In, RnW, n_RD, n_WE, n_ROMSEL, SoundIn, SoundOut, n_IRQ, n_VRAM_A10, n_VRAM_CS, D_Out, PD_Out
  LS139 U3_DoubleDMX ();  // open: n_EN1, n_EN2, A1_0, A1_1, A2_0, A2_1, n_Y1, n_Y2
  PPU ppu_inst ();  // open: CLK, n_RST, RS0, RS1, RS2, n_DBE, D_In, AD_In, EXT_In, ALE, n_INT, n_RD, n_WE, VIDEO, D_Out, AD_Out, AHi_Out, EXT_Out
  P3 tv_port ();  // open: AUDIO, VIDEO
  LS373 U2_Latch ();  // open: LE, n_OE, D, Q
endmodule

module APU (
  input  CLK,
  input  [7:0] D_In,
  input  n_IN0,
  input  n_IN1,
  input  n_NMI,
  input  n_RST,
  input  n_IRQ,
  output [7:0] D_Out,
  output OUT_0,
  output OUT_1,
  output OUT_2,
  output AUX_A,
  output AUX_B,
  output M2,
  output [15:0] A_Out,
  output RnW
);
endmodule

module PPU (
  input  CLK,
  input  n_RST,
  input  RS0,
  input  RS1,
  input  RS2,
  input  n_DBE,
  input  [7:0] D_In,
  input  [7:0] AD_In,
  input  [3:0] EXT_In,
  output ALE,
  output n_INT,
  output n_RD,
  output n_WE,
  output VIDEO,
  output [7:0] D_Out,
  output [7:0] AD_Out,
  output [5:0] AHi_Out,
  output [3:0] EXT_Out
);
endmodule

module U_40H368 (
  input  n_G1,
  input  n_G2,
  input  A1,
  input  A2,
  input  A3,
  input  A4,
  input  A5,
  input  A6,
  output Y1,
  output Y2,
  output Y3,
  output Y4,
  output Y5,
  output Y6
);

  wire not_1_out, not_2_out;

  not not_1 (not_1_out, n_G1);
  not not_2 (not_2_out, n_G2);
  assign Y1 = not_1_out ? ~A1 : 1'bz;  // Controlled_Inverter controlled_inverter_1
  assign Y2 = not_1_out ? ~A2 : 1'bz;  // Controlled_Inverter controlled_inverter_2
  assign Y3 = not_1_out ? ~A3 : 1'bz;  // Controlled_Inverter controlled_inverter_3
  assign Y4 = not_1_out ? ~A4 : 1'bz;  // Controlled_Inverter controlled_inverter_4
  assign Y5 = not_2_out ? ~A5 : 1'bz;  // Controlled_Inverter controlled_inverter_5
  assign Y6 = not_2_out ? ~A6 : 1'bz;  // Controlled_Inverter controlled_inverter_6

  // Notes on the sheet:
  //   40H368
endmodule

module P1 (
  input  [14:0] A_In,
  input  M2,
  input  [13:0] PA_In,
  input  n_PA13,
  input  [7:0] D_In,
  input  [7:0] PD_In,
  input  RnW,
  input  n_RD,
  input  n_WE,
  input  n_ROMSEL,
  input  SoundIn,
  output SoundOut,
  output n_IRQ,
  output n_VRAM_A10,
  output n_VRAM_CS,
  output [7:0] D_Out,
  output [7:0] PD_Out
);
endmodule

module P2 (
  input  S4017_CUP,
  input  OUT_2,
  input  OUT_1,
  input  OUT_0,
  input  S4016_CUP,
  output SOUND,
  output n_IRQ,
  output S4017_D4,
  output S4017_D3,
  output S4017_D2,
  output S4017_D1,
  output S4017_D0,
  output S4016_D1
);
endmodule

module P3 (
  input  AUDIO,
  input  VIDEO
);
endmodule

module P4 (
  input  OUT_0,
  input  S4016_CUP,
  output S4016_D0
);
endmodule

module P5 (
  input  OUT_0,
  input  S4017_CUP,
  output S4017_D0,
  output MIC
);
endmodule

module LS139 (
  input  n_EN1,
  input  n_EN2,
  input  A1_0,
  input  A1_1,
  input  A2_0,
  input  A2_1,
  output [3:0] n_Y1,
  output [3:0] n_Y2
);

  wire nand_1_out, nand_2_out, nand_3_out, nand_4_out, nand_5_out, nand_6_out, nand_7_out, nand_8_out,
       not_1_out, not_2_out, not_3_out, not_4_out, not_5_out, not_6_out, not_7_out, not_8_out, not_9_out,
       not_10_out, not_11_out, not_12_out, not_13_out, not_14_out, not_15_out, not_16_out, not_17_out,
       not_18_out;

  not not_1 (not_1_out, n_EN1);
  not not_2 (not_2_out, n_EN2);
  not not_3 (not_3_out, A1_0);
  not not_4 (not_4_out, A1_1);
  not not_5 (not_5_out, A2_0);
  not not_6 (not_6_out, A2_1);
  not not_7 (not_7_out, not_3_out);
  not not_8 (not_8_out, not_4_out);
  not not_9 (not_9_out, not_5_out);
  not not_10 (not_10_out, not_6_out);
  nand nand_1 (nand_1_out, not_3_out, not_4_out, not_1_out);
  not not_11 (not_11_out, nand_1_out);
  nand nand_2 (nand_2_out, not_7_out, not_4_out, not_1_out);
  not not_12 (not_12_out, nand_2_out);
  nand nand_3 (nand_3_out, not_3_out, not_8_out, not_1_out);
  not not_13 (not_13_out, nand_3_out);
  nand nand_4 (nand_4_out, not_7_out, not_8_out, not_1_out);
  not not_14 (not_14_out, nand_4_out);
  nand nand_5 (nand_5_out, not_5_out, not_6_out, not_2_out);
  not not_15 (not_15_out, nand_5_out);
  nand nand_6 (nand_6_out, not_9_out, not_6_out, not_2_out);
  not not_16 (not_16_out, nand_6_out);
  nand nand_7 (nand_7_out, not_5_out, not_10_out, not_2_out);
  not not_17 (not_17_out, nand_7_out);
  nand nand_8 (nand_8_out, not_9_out, not_10_out, not_2_out);
  not not_18 (not_18_out, nand_8_out);
  not not_19 (n_Y1[0], not_11_out);
  not not_20 (n_Y1[1], not_12_out);
  not not_21 (n_Y1[2], not_13_out);
  not not_22 (n_Y1[3], not_14_out);
  not not_23 (n_Y2[0], not_15_out);
  not not_24 (n_Y2[1], not_16_out);
  not not_25 (n_Y2[2], not_17_out);
  not not_26 (n_Y2[3], not_18_out);

  // Notes on the sheet:
  //   Double inverting 2-DMX with #Enabler
endmodule

module LS373 (
  input  LE,
  input  n_OE,
  input  [7:0] D,
  output [7:0] Q
);

  wire not_1_out, not_2_out, not_3_out;
  wire [7:0] ls373_latch_1_q;

  not not_1 (not_1_out, LE);
  not not_2 (not_2_out, n_OE);
  not not_3 (not_3_out, not_1_out);
  LS373_Latch ls373_latch_1 (.LE(not_3_out), .n_LE(not_1_out), .D(D[0]), .Q(ls373_latch_1_q[0]));
  LS373_Latch ls373_latch_2 (.LE(not_3_out), .n_LE(not_1_out), .D(D[1]), .Q(ls373_latch_1_q[1]));
  LS373_Latch ls373_latch_3 (.LE(not_3_out), .n_LE(not_1_out), .D(D[2]), .Q(ls373_latch_1_q[2]));
  LS373_Latch ls373_latch_4 (.LE(not_3_out), .n_LE(not_1_out), .D(D[3]), .Q(ls373_latch_1_q[3]));
  LS373_Latch ls373_latch_5 (.LE(not_3_out), .n_LE(not_1_out), .D(D[4]), .Q(ls373_latch_1_q[4]));
  LS373_Latch ls373_latch_6 (.LE(not_3_out), .n_LE(not_1_out), .D(D[5]), .Q(ls373_latch_1_q[5]));
  LS373_Latch ls373_latch_7 (.LE(not_3_out), .n_LE(not_1_out), .D(D[6]), .Q(ls373_latch_1_q[6]));
  LS373_Latch ls373_latch_8 (.LE(not_3_out), .n_LE(not_1_out), .D(D[7]), .Q(ls373_latch_1_q[7]));
  assign Q = not_2_out ? ls373_latch_1_q : 8'bz;  // Controlled_Buffer controlled_buffer_1

  // Notes on the sheet:
  //   Octal D-type transparent latch; 3-state
endmodule

module S_RAM (
  input  in_1
);
endmodule

module LS373_Latch (
  input  LE,
  input  n_LE,
  input  D,
  output Q
);

  wire not_2_out, transmission_1_p2, transmission_1_p3, transmission_1_p4, transmission_1_p7,
       transmission_2_p1, transmission_2_p6;

  // Transmission_Gate transmission_1: pin names not known; wires that end beside it: n_LE, transmission_1_p2, transmission_1_p3, transmission_1_p4, transmission_1_p2, transmission_1_p3, transmission_1_p7, transmission_1_p2, transmission_1_p3
  // Transmission_Gate transmission_2: pin names not known; wires that end beside it: transmission_2_p1, transmission_2_p1, transmission_1_p3, transmission_1_p2, transmission_1_p4, transmission_2_p6
  D_Flip_Flop #(.trigger("high")) d_ff_1 (.D(D), .clk(LE), .Q(Q));  // open: Qn, preset, reset
  not not_1 (transmission_1_p7, not_2_out);
  not not_2 (not_2_out, transmission_1_p4);
  not not_3 (transmission_2_p6, not_2_out);

  // Notes on the sheet:
  //   LE
  //   ~LE
  //   D
  //   Q
endmodule
