// Logisim project 2C04 PPU RGB OUT.circ as structural Verilog: 8 circuits, main circuit main
module main (
);

  wire clock_1_out, counter_1_carry, rgb_out_1_sync_2;
  wire [5:0] counter_1_q;
  wire [23:0] rgb_out_1_r;

  Counter #(.width(6), .max('h3f)) counter_1 (
    .count(1'b1), .Q(counter_1_q), .carry(counter_1_carry), .clk(clock_1_out));  // open: load, D, clr
  Clock clock_1 (.out(clock_1_out));
  RGB_OUT rgb_out_1 (
    .PCLK(clock_1_out), .R(rgb_out_1_r[0]), .out_14(rgb_out_1_r[1]), .out_15(rgb_out_1_r[2]),
    .out_16(rgb_out_1_r[3]), .out_17(rgb_out_1_r[4]), .out_18(rgb_out_1_r[5]), .out_19(rgb_out_1_r[6]),
    .out_20(rgb_out_1_r[7]), .G(rgb_out_1_r[8]), .out_22(rgb_out_1_r[9]), .out_23(rgb_out_1_r[10]),
    .out_24(rgb_out_1_r[11]), .out_25(rgb_out_1_r[12]), .out_26(rgb_out_1_r[13]), .out_27(rgb_out_1_r[14]),
    .out_28(rgb_out_1_r[15]), .B(rgb_out_1_r[16]), .out_30(rgb_out_1_r[17]), .out_31(rgb_out_1_r[18]),
    .out_32(rgb_out_1_r[19]), .out_33(rgb_out_1_r[20]), .out_34(rgb_out_1_r[21]), .out_35(rgb_out_1_r[22]),
    .out_36(rgb_out_1_r[23]), .SYNC_2(rgb_out_1_sync_2), .PICTURE(1'b0), .nTR(1'b1), .nTG(1'b1), .nTB(1'b1),
    .nCC0(counter_1_q[2]), .nCC1(counter_1_q[3]), .nCC2(counter_1_q[4]), .nCC3(counter_1_q[5]),
    .SYNC(counter_1_carry), .nLL0(counter_1_q[0]), .nLL1(counter_1_q[1]));
  RAM #(.addrWidth(6), .dataWidth(24)) ram_1 (
    .addr(counter_1_q), .data(rgb_out_1_r), .sel(1'b1), .clk(clock_1_out), .ld(1'b0));  // open: clr
endmodule

module D_LATCH (
  input  EN,
  input  D,
  output Q,
  output nQ
);

  D_Flip_Flop d_ff_1 (.clk(EN), .D(D), .Q(Q), .Qn(nQ));  // open: preset, en, reset
endmodule

// RGB OUT
module RGB_OUT (
  input  PCLK,
  input  PICTURE,
  input  nTR,
  input  nTG,
  input  nTB,
  input  nCC0,
  input  nCC1,
  input  nCC2,
  input  nCC3,
  input  nLL0,
  input  nLL1,
  input  SYNC,
  output R,
  output out_14,
  output out_15,
  output out_16,
  output out_17,
  output out_18,
  output out_19,
  output out_20,
  output G,
  output out_22,
  output out_23,
  output out_24,
  output out_25,
  output out_26,
  output out_27,
  output out_28,
  output B,
  output out_30,
  output out_31,
  output out_32,
  output out_33,
  output out_34,
  output out_35,
  output out_36,
  output SYNC_2
);

  wire and_1_out, and_2_out, and_3_out, and_4_out, and_5_out, and_6_out, and_7_out, and_8_out, and_9_out,
       d_latch_1_nq, d_latch_2_nq, d_latch_3_nq, d_latch_4_nq, d_latch_5_nq, d_latch_6_nq, d_latch_7_nq,
       d_latch_8_nq, d_latch_15_nq, nor_1_out, nor_2_out, nor_3_out, nor_4_out, nor_5_out, nor_6_out,
       nor_7_out, nor_8_out, nor_9_out, nor_10_out, nor_11_out, nor_12_out, nor_13_out, nor_14_out,
       nor_15_out, nor_16_out, nor_17_out, nor_18_out, nor_19_out, nor_20_out, nor_21_out, nor_22_out,
       nor_23_out, nor_24_out, nor_25_out, nor_26_out, nor_27_out, nor_28_out, not_1_out, not_2_out,
       not_3_out, not_4_out, not_5_out, not_6_out, not_7_out, not_8_out, not_9_out, not_10_out, not_11_out,
       not_12_out, sel4x16_1__0, sel4x16_1__1, sel4x16_1__2, sel4x16_1__3, sel4x16_1__4, sel4x16_1__5,
       sel4x16_1__6, sel4x16_1__7, sel4x16_1__8, sel4x16_1__9, sel4x16_1__10, sel4x16_1__11, sel4x16_1__12,
       sel4x16_1__13, sel4x16_1__14, sel4x16_1__15, sel_12x3_1_out0, sel_12x3_1_out1, sel_12x3_1_out2,
       sel_12x3_2_out0, sel_12x3_2_out1, sel_12x3_2_out2, sel_12x3_3_out0, sel_12x3_3_out1, sel_12x3_3_out2,
       sel_16x12_b_1_out0, sel_16x12_b_1_out1, sel_16x12_b_1_out2, sel_16x12_b_1_out3, sel_16x12_b_1_out4,
       sel_16x12_b_1_out5, sel_16x12_b_1_out6, sel_16x12_b_1_out7, sel_16x12_b_1_out8, sel_16x12_b_1_out9,
       sel_16x12_b_1_out10, sel_16x12_b_1_out11, sel_16x12_g_1_out0, sel_16x12_g_1_out1, sel_16x12_g_1_out2,
       sel_16x12_g_1_out3, sel_16x12_g_1_out4, sel_16x12_g_1_out5, sel_16x12_g_1_out6, sel_16x12_g_1_out7,
       sel_16x12_g_1_out8, sel_16x12_g_1_out9, sel_16x12_g_1_out10, sel_16x12_g_1_out11, sel_16x12_r_1_out0,
       sel_16x12_r_1_out1, sel_16x12_r_1_out2, sel_16x12_r_1_out3, sel_16x12_r_1_out4, sel_16x12_r_1_out5,
       sel_16x12_r_1_out6, sel_16x12_r_1_out7, sel_16x12_r_1_out8, sel_16x12_r_1_out9, sel_16x12_r_1_out10,
       sel_16x12_r_1_out11;

  D_LATCH d_latch_1 (.EN(not_1_out), .D(SYNC), .nQ(d_latch_1_nq));  // open: Q
  not not_1 (not_1_out, PCLK);
  D_LATCH d_latch_2 (.EN(PCLK), .nQ(d_latch_2_nq));  // open: D, Q
  D_LATCH d_latch_3 (.EN(PCLK), .nQ(d_latch_3_nq));  // open: D, Q
  D_LATCH d_latch_4 (.EN(PCLK), .nQ(d_latch_4_nq));  // open: D, Q
  D_LATCH d_latch_5 (.EN(PCLK), .nQ(d_latch_5_nq));  // open: D, Q
  D_LATCH d_latch_6 (.EN(PCLK), .nQ(d_latch_6_nq));  // open: D, Q
  D_LATCH d_latch_7 (.EN(PCLK), .nQ(d_latch_7_nq));  // open: D, Q
  D_LATCH d_latch_8 (.EN(PCLK), .D(d_latch_1_nq), .nQ(d_latch_8_nq));  // open: Q
  D_LATCH d_latch_9 (.EN(not_1_out), .D(d_latch_2_nq));  // open: Q, nQ
  D_LATCH d_latch_10 (.EN(not_1_out), .D(d_latch_3_nq));  // open: Q, nQ
  D_LATCH d_latch_11 (.EN(not_1_out), .D(d_latch_4_nq));  // open: Q, nQ
  D_LATCH d_latch_12 (.EN(not_1_out), .D(d_latch_5_nq));  // open: Q, nQ
  D_LATCH d_latch_13 (.EN(not_1_out), .D(d_latch_6_nq));  // open: Q, nQ
  D_LATCH d_latch_14 (.EN(not_1_out), .D(d_latch_7_nq));  // open: Q, nQ
  D_LATCH d_latch_15 (.EN(not_1_out), .D(d_latch_8_nq), .nQ(d_latch_15_nq));  // open: Q
  SEL4x16 sel4x16_1 (
    ._15(sel4x16_1__15), ._14(sel4x16_1__14), ._13(sel4x16_1__13), ._12(sel4x16_1__12), ._11(sel4x16_1__11),
    ._10(sel4x16_1__10), ._9(sel4x16_1__9), ._8(sel4x16_1__8), ._7(sel4x16_1__7), ._6(sel4x16_1__6),
    ._5(sel4x16_1__5), ._4(sel4x16_1__4), .C2(nCC2), .C3(nCC3), .L0(nLL0), .L1(nLL1), ._3(sel4x16_1__3),
    ._2(sel4x16_1__2), ._1(sel4x16_1__1), ._0(sel4x16_1__0), .PCLK(PCLK));
  SEL_16x12_R sel_16x12_r_1 (
    .OUT0(sel_16x12_r_1_out0), .OUT1(sel_16x12_r_1_out1), .OUT2(sel_16x12_r_1_out2),
    .OUT3(sel_16x12_r_1_out3), .OUT4(sel_16x12_r_1_out4), .OUT5(sel_16x12_r_1_out5),
    .OUT6(sel_16x12_r_1_out6), .OUT7(sel_16x12_r_1_out7), .OUT8(sel_16x12_r_1_out8),
    .OUT9(sel_16x12_r_1_out9), .OUT10(sel_16x12_r_1_out10), .OUT11(sel_16x12_r_1_out11), ._15(sel4x16_1__15),
    ._14(sel4x16_1__14), ._13(sel4x16_1__13), ._12(sel4x16_1__12), ._11(sel4x16_1__11), ._10(sel4x16_1__10),
    ._9(sel4x16_1__9), ._8(sel4x16_1__8), ._7(sel4x16_1__7), ._6(sel4x16_1__6), ._5(sel4x16_1__5),
    ._4(sel4x16_1__4), ._3(sel4x16_1__3), ._2(sel4x16_1__2), ._1(sel4x16_1__1), ._0(sel4x16_1__0), .PCLK(PCLK));
  SEL_16x12_G sel_16x12_g_1 (
    .PCLK(PCLK), ._15(sel4x16_1__15), ._14(sel4x16_1__14), ._13(sel4x16_1__13), ._12(sel4x16_1__12),
    ._11(sel4x16_1__11), ._10(sel4x16_1__10), ._9(sel4x16_1__9), ._8(sel4x16_1__8), ._7(sel4x16_1__7),
    ._6(sel4x16_1__6), ._5(sel4x16_1__5), ._4(sel4x16_1__4), ._3(sel4x16_1__3), ._2(sel4x16_1__2),
    ._1(sel4x16_1__1), ._0(sel4x16_1__0), .OUT0(sel_16x12_g_1_out0), .OUT1(sel_16x12_g_1_out1),
    .OUT2(sel_16x12_g_1_out2), .OUT3(sel_16x12_g_1_out3), .OUT4(sel_16x12_g_1_out4),
    .OUT5(sel_16x12_g_1_out5), .OUT6(sel_16x12_g_1_out6), .OUT7(sel_16x12_g_1_out7),
    .OUT8(sel_16x12_g_1_out8), .OUT9(sel_16x12_g_1_out9), .OUT10(sel_16x12_g_1_out10),
    .OUT11(sel_16x12_g_1_out11));
  SEL_16x12_B sel_16x12_b_1 (
    .PCLK(PCLK), ._15(sel4x16_1__15), ._14(sel4x16_1__14), ._13(sel4x16_1__13), ._12(sel4x16_1__12),
    ._11(sel4x16_1__11), ._10(sel4x16_1__10), ._9(sel4x16_1__9), ._8(sel4x16_1__8), ._7(sel4x16_1__7),
    ._6(sel4x16_1__6), ._5(sel4x16_1__5), ._4(sel4x16_1__4), ._3(sel4x16_1__3), ._2(sel4x16_1__2),
    ._1(sel4x16_1__1), ._0(sel4x16_1__0), .OUT0(sel_16x12_b_1_out0), .OUT1(sel_16x12_b_1_out1),
    .OUT2(sel_16x12_b_1_out2), .OUT3(sel_16x12_b_1_out3), .OUT4(sel_16x12_b_1_out4),
    .OUT5(sel_16x12_b_1_out5), .OUT6(sel_16x12_b_1_out6), .OUT7(sel_16x12_b_1_out7),
    .OUT8(sel_16x12_b_1_out8), .OUT9(sel_16x12_b_1_out9), .OUT10(sel_16x12_b_1_out10),
    .OUT11(sel_16x12_b_1_out11));
  nor nor_1 (nor_1_out, not_1_out, nCC1, not_2_out);
  not not_2 (not_2_out, nCC0);
  not not_3 (not_3_out, nCC1);
  SEL_12x3 sel_12x3_1 (
    .IN0(sel_16x12_r_1_out0), .IN1(sel_16x12_r_1_out1), .IN2(sel_16x12_r_1_out2), .IN3(sel_16x12_r_1_out3),
    .IN4(sel_16x12_r_1_out4), .IN5(sel_16x12_r_1_out5), .IN6(sel_16x12_r_1_out6), .IN7(sel_16x12_r_1_out7),
    .IN8(sel_16x12_r_1_out8), .IN9(sel_16x12_r_1_out9), .IN10(sel_16x12_r_1_out10),
    .IN11(sel_16x12_r_1_out11), .OUT0(sel_12x3_1_out0), .OUT1(sel_12x3_1_out1), .OUT2(sel_12x3_1_out2),
    ._1(nor_1_out), ._2(nor_2_out), ._3(nor_3_out), ._4(nor_4_out), .nTx(nTR), .PCLK(PCLK));
  SEL_12x3 sel_12x3_2 (
    .IN0(sel_16x12_g_1_out0), .IN1(sel_16x12_g_1_out1), .IN2(sel_16x12_g_1_out2), .IN3(sel_16x12_g_1_out3),
    .IN4(sel_16x12_g_1_out4), .IN5(sel_16x12_g_1_out5), .IN6(sel_16x12_g_1_out6), .IN7(sel_16x12_g_1_out7),
    .IN8(sel_16x12_g_1_out8), .IN9(sel_16x12_g_1_out9), .IN10(sel_16x12_g_1_out10),
    .IN11(sel_16x12_g_1_out11), .OUT0(sel_12x3_2_out0), .OUT1(sel_12x3_2_out1), .OUT2(sel_12x3_2_out2),
    ._1(nor_1_out), ._2(nor_2_out), ._3(nor_3_out), ._4(nor_4_out), .nTx(nTG), .PCLK(PCLK));
  SEL_12x3 sel_12x3_3 (
    .IN0(sel_16x12_b_1_out0), .IN1(sel_16x12_b_1_out1), .IN2(sel_16x12_b_1_out2), .IN3(sel_16x12_b_1_out3),
    .IN4(sel_16x12_b_1_out4), .IN5(sel_16x12_b_1_out5), .IN6(sel_16x12_b_1_out6), .IN7(sel_16x12_b_1_out7),
    .IN8(sel_16x12_b_1_out8), .IN9(sel_16x12_b_1_out9), .IN10(sel_16x12_b_1_out10),
    .IN11(sel_16x12_b_1_out11), .OUT0(sel_12x3_3_out0), .OUT1(sel_12x3_3_out1), .OUT2(sel_12x3_3_out2),
    ._1(nor_1_out), ._2(nor_2_out), ._3(nor_3_out), ._4(nor_4_out), .nTx(nTB), .PCLK(PCLK));
  nor nor_2 (nor_2_out, not_1_out, nCC1, nCC0);
  nor nor_3 (nor_3_out, not_1_out, not_3_out, not_2_out);
  and and_1 (and_1_out, ~PICTURE, sel_12x3_1_out2);  // AND_Gate
  and and_2 (and_2_out, ~PICTURE, sel_12x3_1_out1);  // AND_Gate
  and and_3 (and_3_out, ~PICTURE, sel_12x3_1_out0);  // AND_Gate
  and and_4 (and_4_out, ~PICTURE, sel_12x3_2_out2);  // AND_Gate
  and and_5 (and_5_out, ~PICTURE, sel_12x3_2_out1);  // AND_Gate
  and and_6 (and_6_out, ~PICTURE, sel_12x3_2_out0);  // AND_Gate
  and and_7 (and_7_out, ~PICTURE, sel_12x3_3_out2);  // AND_Gate
  and and_8 (and_8_out, ~PICTURE, sel_12x3_3_out1);  // AND_Gate
  and and_9 (and_9_out, ~PICTURE, sel_12x3_3_out0);  // AND_Gate
  nor nor_4 (nor_4_out, not_1_out, not_3_out, nCC0);
  not not_4 (not_4_out, and_2_out);
  not not_5 (not_5_out, and_3_out);
  not not_6 (not_6_out, and_5_out);
  not not_7 (not_7_out, and_6_out);
  not not_8 (not_8_out, and_9_out);
  not not_9 (not_9_out, and_8_out);
  not not_10 (not_10_out, and_1_out);
  not not_11 (not_11_out, and_4_out);
  not not_12 (not_12_out, and_7_out);
  nor nor_5 (nor_5_out, and_3_out, and_2_out, and_1_out);
  nor nor_6 (nor_6_out, not_5_out, and_2_out, and_1_out);
  nor nor_7 (nor_7_out, and_3_out, not_4_out, and_1_out);
  nor nor_8 (nor_8_out, not_5_out, not_4_out, and_1_out);
  nor nor_9 (nor_9_out, and_3_out, and_2_out, not_10_out);
  nor nor_10 (nor_10_out, not_5_out, and_2_out, not_10_out);
  nor nor_11 (nor_11_out, and_3_out, not_4_out, not_10_out);
  nor nor_12 (nor_12_out, not_5_out, not_4_out, not_10_out);
  nor nor_13 (nor_13_out, and_6_out, and_5_out, and_4_out);
  nor nor_14 (nor_14_out, not_7_out, and_5_out, and_4_out);
  nor nor_15 (nor_15_out, and_6_out, not_6_out, and_4_out);
  nor nor_16 (nor_16_out, not_7_out, not_6_out, and_4_out);
  nor nor_17 (nor_17_out, and_6_out, and_5_out, not_11_out);
  nor nor_18 (nor_18_out, not_7_out, and_5_out, not_11_out);
  nor nor_19 (nor_19_out, and_6_out, not_6_out, not_11_out);
  nor nor_20 (nor_20_out, not_7_out, not_6_out, not_11_out);
  nor nor_21 (nor_21_out, and_9_out, and_8_out, and_7_out);
  nor nor_22 (nor_22_out, not_8_out, and_8_out, and_7_out);
  nor nor_23 (nor_23_out, and_9_out, not_9_out, and_7_out);
  nor nor_24 (nor_24_out, not_8_out, not_9_out, and_7_out);
  nor nor_25 (nor_25_out, and_9_out, and_8_out, not_12_out);
  nor nor_26 (nor_26_out, not_8_out, and_8_out, not_12_out);
  nor nor_27 (nor_27_out, and_9_out, not_9_out, not_12_out);
  nor nor_28 (nor_28_out, not_8_out, not_9_out, not_12_out);
  D_LATCH d_latch_16 (.EN(not_1_out), .D(nor_5_out), .Q(R));  // open: nQ
  D_LATCH d_latch_17 (.EN(not_1_out), .D(nor_6_out), .Q(out_14));  // open: nQ
  D_LATCH d_latch_18 (.EN(not_1_out), .D(nor_7_out), .Q(out_15));  // open: nQ
  D_LATCH d_latch_19 (.EN(not_1_out), .D(nor_8_out), .Q(out_16));  // open: nQ
  D_LATCH d_latch_20 (.EN(not_1_out), .D(nor_9_out), .Q(out_17));  // open: nQ
  D_LATCH d_latch_21 (.EN(not_1_out), .D(nor_10_out), .Q(out_18));  // open: nQ
  D_LATCH d_latch_22 (.EN(not_1_out), .D(nor_11_out), .Q(out_19));  // open: nQ
  D_LATCH d_latch_23 (.EN(not_1_out), .D(nor_12_out), .Q(out_20));  // open: nQ
  D_LATCH d_latch_24 (.EN(not_1_out), .D(nor_13_out), .Q(G));  // open: nQ
  D_LATCH d_latch_25 (.EN(not_1_out), .D(nor_14_out), .Q(out_22));  // open: nQ
  D_LATCH d_latch_26 (.EN(not_1_out), .D(nor_15_out), .Q(out_23));  // open: nQ
  D_LATCH d_latch_27 (.EN(not_1_out), .D(nor_16_out), .Q(out_24));  // open: nQ
  D_LATCH d_latch_28 (.EN(not_1_out), .D(nor_17_out), .Q(out_25));  // open: nQ
  D_LATCH d_latch_29 (.EN(not_1_out), .D(nor_18_out), .Q(out_26));  // open: nQ
  D_LATCH d_latch_30 (.EN(not_1_out), .D(nor_19_out), .Q(out_27));  // open: nQ
  D_LATCH d_latch_31 (.EN(not_1_out), .D(nor_20_out), .Q(out_28));  // open: nQ
  D_LATCH d_latch_32 (.EN(not_1_out), .D(nor_21_out), .Q(B));  // open: nQ
  D_LATCH d_latch_33 (.EN(not_1_out), .D(nor_22_out), .Q(out_30));  // open: nQ
  D_LATCH d_latch_34 (.EN(not_1_out), .D(nor_23_out), .Q(out_31));  // open: nQ
  D_LATCH d_latch_35 (.EN(not_1_out), .D(nor_24_out), .Q(out_32));  // open: nQ
  D_LATCH d_latch_36 (.EN(not_1_out), .D(nor_25_out), .Q(out_33));  // open: nQ
  D_LATCH d_latch_37 (.EN(not_1_out), .D(nor_26_out), .Q(out_34));  // open: nQ
  D_LATCH d_latch_38 (.EN(not_1_out), .D(nor_27_out), .Q(out_35));  // open: nQ
  D_LATCH d_latch_39 (.EN(not_1_out), .D(nor_28_out), .Q(out_36));  // open: nQ
  not not_13 (SYNC_2, d_latch_15_nq);

  // Notes on the sheet:
  //   1
  //   2
  //   3
  //   4
  //   2
  //   1
  //   0
  //   2
  //   1
  //   0
  //   2
  //   1
  //   0
endmodule

module SEL_12x3 (
  input  PCLK,
  input  nTx,
  input  IN0,
  input  IN1,
  input  IN2,
  input  IN3,
  input  IN4,
  input  IN5,
  input  IN6,
  input  IN7,
  input  IN8,
  input  IN9,
  input  IN10,
  input  IN11,
  input  _1,
  input  _2,
  input  _3,
  input  _4,
  output OUT2,
  output OUT1,
  output OUT0
);

  wire and_1_out, and_2_out, and_3_out, and_4_out, and_5_out, and_6_out, and_7_out, and_8_out, and_9_out,
       and_10_out, and_11_out, and_12_out, not_1_out, or_1_out, or_2_out, or_3_out;

  not not_1 (not_1_out, nTx);
  and and_1 (and_1_out, IN0, _2);
  and and_2 (and_2_out, IN1, _4);
  and and_3 (and_3_out, IN2, _1);
  and and_4 (and_4_out, IN3, _3);
  and and_5 (and_5_out, IN4, _2);
  and and_6 (and_6_out, IN5, _4);
  and and_7 (and_7_out, IN6, _1);
  and and_8 (and_8_out, IN7, _3);
  and and_9 (and_9_out, IN8, _2);
  and and_10 (and_10_out, IN9, _4);
  and and_11 (and_11_out, IN10, _1);
  and and_12 (and_12_out, IN11, _3);
  or or_1 (or_1_out, and_1_out, and_2_out, and_3_out, and_4_out);
  or or_2 (or_2_out, and_5_out, and_6_out, and_7_out, and_8_out);
  or or_3 (or_3_out, and_9_out, and_10_out, and_11_out, and_12_out);
  D_Flip_Flop #(.trigger("low")) d_ff_1 (
    .clk(PCLK), .D(or_1_out), .Q(OUT2), .reset(not_1_out));  // open: Qn, preset, en
  D_Flip_Flop #(.trigger("low")) d_ff_2 (
    .clk(PCLK), .D(or_2_out), .Q(OUT1), .reset(not_1_out));  // open: Qn, preset, en
  D_Flip_Flop #(.trigger("low")) d_ff_3 (
    .clk(PCLK), .D(or_3_out), .Q(OUT0), .reset(not_1_out));  // open: Qn, preset, en
endmodule

module SEL_16x12_R (
  input  PCLK,
  input  _15,
  input  _14,
  input  _13,
  input  _12,
  input  _11,
  input  _10,
  input  _9,
  input  _8,
  input  _7,
  input  _6,
  input  _5,
  input  _4,
  input  _3,
  input  _2,
  input  _1,
  input  _0,
  output OUT0,
  output OUT1,
  output OUT2,
  output OUT3,
  output OUT4,
  output OUT5,
  output OUT6,
  output OUT7,
  output OUT8,
  output OUT9,
  output OUT10,
  output OUT11
);

  wire not_1_out, transistor_1_out, transistor_2_out, transistor_3_out, transistor_5_out, transistor_7_out,
       transistor_9_out, transistor_10_out, transistor_12_out, transistor_15_out, transistor_17_out,
       transistor_18_out, transistor_34_out;

  not not_1 (not_1_out, PCLK);
  and and_1 (OUT0, not_1_out, transistor_1_out);
  and and_2 (OUT1, not_1_out, transistor_12_out);
  and and_3 (OUT2, not_1_out, transistor_34_out);
  and and_4 (OUT3, not_1_out, transistor_2_out);
  and and_5 (OUT4, not_1_out, transistor_3_out);
  and and_6 (OUT5, not_1_out, transistor_15_out);
  and and_7 (OUT6, not_1_out, transistor_5_out);
  and and_8 (OUT7, not_1_out, transistor_7_out);
  and and_9 (OUT8, not_1_out, transistor_17_out);
  and and_10 (OUT9, not_1_out, transistor_18_out);
  and and_11 (OUT10, not_1_out, transistor_9_out);
  and and_12 (OUT11, not_1_out, transistor_10_out);
  Transistor #(.\type ("n")) transistor_1 (.in(1'b0), .out(transistor_1_out), .gate(_14));
  Transistor #(.\type ("n")) transistor_2 (.in(1'b0), .out(transistor_2_out), .gate(_14));
  Transistor #(.\type ("n")) transistor_3 (.in(1'b0), .out(transistor_3_out), .gate(_14));
  Transistor #(.\type ("n")) transistor_4 (.in(1'b0), .out(transistor_3_out), .gate(_15));
  Transistor #(.\type ("n")) transistor_5 (.in(1'b0), .out(transistor_5_out), .gate(_14));
  Transistor #(.\type ("n")) transistor_6 (.in(1'b0), .out(transistor_5_out), .gate(_15));
  Transistor #(.\type ("n")) transistor_7 (.in(1'b0), .out(transistor_7_out), .gate(_14));
  Transistor #(.\type ("n")) transistor_8 (.in(1'b0), .out(transistor_7_out), .gate(_15));
  Transistor #(.\type ("n")) transistor_9 (.in(1'b0), .out(transistor_9_out), .gate(_15));
  Transistor #(.\type ("n")) transistor_10 (.in(1'b0), .out(transistor_10_out), .gate(_14));
  Transistor #(.\type ("n")) transistor_11 (.in(1'b0), .out(transistor_1_out), .gate(_13));
  Transistor #(.\type ("n")) transistor_12 (.in(1'b0), .out(transistor_12_out), .gate(_13));
  Transistor #(.\type ("n")) transistor_13 (.in(1'b0), .out(transistor_2_out), .gate(_13));
  Transistor #(.\type ("n")) transistor_14 (.in(1'b0), .out(transistor_3_out), .gate(_12));
  Transistor #(.\type ("n")) transistor_15 (.in(1'b0), .out(transistor_15_out), .gate(_13));
  Transistor #(.\type ("n")) transistor_16 (.in(1'b0), .out(transistor_7_out), .gate(_13));
  Transistor #(.\type ("n")) transistor_17 (.in(1'b0), .out(transistor_17_out), .gate(_12));
  Transistor #(.\type ("n")) transistor_18 (.in(1'b0), .out(transistor_18_out), .gate(_12));
  Transistor #(.\type ("n")) transistor_19 (.in(1'b0), .out(transistor_18_out), .gate(_13));
  Transistor #(.\type ("n")) transistor_20 (.in(1'b0), .out(transistor_9_out), .gate(_12));
  Transistor #(.\type ("n")) transistor_21 (.in(1'b0), .out(transistor_10_out), .gate(_13));
  Transistor #(.\type ("n")) transistor_22 (.in(1'b0), .out(transistor_1_out), .gate(_11));
  Transistor #(.\type ("n")) transistor_23 (.in(1'b0), .out(transistor_12_out), .gate(_11));
  Transistor #(.\type ("n")) transistor_24 (.in(1'b0), .out(transistor_3_out), .gate(_11));
  Transistor #(.\type ("n")) transistor_25 (.in(1'b0), .out(transistor_15_out), .gate(_11));
  Transistor #(.\type ("n")) transistor_26 (.in(1'b0), .out(transistor_5_out), .gate(_11));
  Transistor #(.\type ("n")) transistor_27 (.in(1'b0), .out(transistor_7_out), .gate(_11));
  Transistor #(.\type ("n")) transistor_28 (.in(1'b0), .out(transistor_17_out), .gate(_11));
  Transistor #(.\type ("n")) transistor_29 (.in(1'b0), .out(transistor_18_out), .gate(_11));
  Transistor #(.\type ("n")) transistor_30 (.in(1'b0), .out(transistor_10_out), .gate(_11));
  Transistor #(.\type ("n")) transistor_31 (.in(1'b0), .out(transistor_1_out), .gate(_10));
  Transistor #(.\type ("n")) transistor_32 (.in(1'b0), .out(transistor_1_out), .gate(_9));
  Transistor #(.\type ("n")) transistor_33 (.in(1'b0), .out(transistor_12_out), .gate(_9));
  Transistor #(.\type ("n")) transistor_34 (.in(1'b0), .out(transistor_34_out), .gate(_9));
  Transistor #(.\type ("n")) transistor_35 (.in(1'b0), .out(transistor_2_out), .gate(_9));
  Transistor #(.\type ("n")) transistor_36 (.in(1'b0), .out(transistor_2_out), .gate(_10));
  Transistor #(.\type ("n")) transistor_37 (.in(1'b0), .out(transistor_3_out), .gate(_9));
  Transistor #(.\type ("n")) transistor_38 (.in(1'b0), .out(transistor_3_out), .gate(_10));
  Transistor #(.\type ("n")) transistor_39 (.in(1'b0), .out(transistor_15_out), .gate(_10));
  Transistor #(.\type ("n")) transistor_40 (.in(1'b0), .out(transistor_5_out), .gate(_9));
  Transistor #(.\type ("n")) transistor_41 (.in(1'b0), .out(transistor_7_out), .gate(_10));
  Transistor #(.\type ("n")) transistor_42 (.in(1'b0), .out(transistor_17_out), .gate(_10));
  Transistor #(.\type ("n")) transistor_43 (.in(1'b0), .out(transistor_17_out), .gate(_9));
  Transistor #(.\type ("n")) transistor_44 (.in(1'b0), .out(transistor_18_out), .gate(_10));
  Transistor #(.\type ("n")) transistor_45 (.in(1'b0), .out(transistor_9_out), .gate(_9));
  Transistor #(.\type ("n")) transistor_46 (.in(1'b0), .out(transistor_9_out), .gate(_10));
  Transistor #(.\type ("n")) transistor_47 (.in(1'b0), .out(transistor_15_out), .gate(_8));
  Transistor #(.\type ("n")) transistor_48 (.in(1'b0), .out(transistor_12_out), .gate(_7));
  Transistor #(.\type ("n")) transistor_49 (.in(1'b0), .out(transistor_34_out), .gate(_7));
  Transistor #(.\type ("n")) transistor_50 (.in(1'b0), .out(transistor_2_out), .gate(_6));
  Transistor #(.\type ("n")) transistor_51 (.in(1'b0), .out(transistor_15_out), .gate(_7));
  Transistor #(.\type ("n")) transistor_52 (.in(1'b0), .out(transistor_5_out), .gate(_7));
  Transistor #(.\type ("n")) transistor_53 (.in(1'b0), .out(transistor_7_out), .gate(_6));
  Transistor #(.\type ("n")) transistor_54 (.in(1'b0), .out(transistor_18_out), .gate(_7));
  Transistor #(.\type ("n")) transistor_55 (.in(1'b0), .out(transistor_9_out), .gate(_7));
  Transistor #(.\type ("n")) transistor_56 (.in(1'b0), .out(transistor_10_out), .gate(_7));
  Transistor #(.\type ("n")) transistor_57 (.in(1'b0), .out(transistor_1_out), .gate(_4));
  Transistor #(.\type ("n")) transistor_58 (.in(1'b0), .out(transistor_34_out), .gate(_5));
  Transistor #(.\type ("n")) transistor_59 (.in(1'b0), .out(transistor_34_out), .gate(_4));
  Transistor #(.\type ("n")) transistor_60 (.in(1'b0), .out(transistor_2_out), .gate(_5));
  Transistor #(.\type ("n")) transistor_61 (.in(1'b0), .out(transistor_2_out), .gate(_4));
  Transistor #(.\type ("n")) transistor_62 (.in(1'b0), .out(transistor_15_out), .gate(_4));
  Transistor #(.\type ("n")) transistor_63 (.in(1'b0), .out(transistor_15_out), .gate(_5));
  Transistor #(.\type ("n")) transistor_64 (.in(1'b0), .out(transistor_5_out), .gate(_4));
  Transistor #(.\type ("n")) transistor_65 (.in(1'b0), .out(transistor_7_out), .gate(_4));
  Transistor #(.\type ("n")) transistor_66 (.in(1'b0), .out(transistor_18_out), .gate(_5));
  Transistor #(.\type ("n")) transistor_67 (.in(1'b0), .out(transistor_18_out), .gate(_4));
  Transistor #(.\type ("n")) transistor_68 (.in(1'b0), .out(transistor_9_out), .gate(_4));
  Transistor #(.\type ("n")) transistor_69 (.in(1'b0), .out(transistor_10_out), .gate(_4));
  Transistor #(.\type ("n")) transistor_70 (.in(1'b0), .out(transistor_12_out), .gate(_3));
  Transistor #(.\type ("n")) transistor_71 (.in(1'b0), .out(transistor_2_out), .gate(_3));
  Transistor #(.\type ("n")) transistor_72 (.in(1'b0), .out(transistor_5_out), .gate(_3));
  Transistor #(.\type ("n")) transistor_73 (.in(1'b0), .out(transistor_7_out), .gate(_3));
  Transistor #(.\type ("n")) transistor_74 (.in(1'b0), .out(transistor_18_out), .gate(_3));
  Transistor #(.\type ("n")) transistor_75 (.in(1'b0), .out(transistor_10_out), .gate(_3));
  Transistor #(.\type ("n")) transistor_76 (.in(1'b0), .out(transistor_1_out), .gate(_2));
  Transistor #(.\type ("n")) transistor_77 (.in(1'b0), .out(transistor_12_out), .gate(_2));
  Transistor #(.\type ("n")) transistor_78 (.in(1'b0), .out(transistor_12_out), .gate(_1));
  Transistor #(.\type ("n")) transistor_79 (.in(1'b0), .out(transistor_2_out), .gate(_1));
  Transistor #(.\type ("n")) transistor_80 (.in(1'b0), .out(transistor_15_out), .gate(_1));
  Transistor #(.\type ("n")) transistor_81 (.in(1'b0), .out(transistor_15_out), .gate(_2));
  Transistor #(.\type ("n")) transistor_82 (.in(1'b0), .out(transistor_7_out), .gate(_1));
  Transistor #(.\type ("n")) transistor_83 (.in(1'b0), .out(transistor_7_out), .gate(_2));
  Transistor #(.\type ("n")) transistor_84 (.in(1'b0), .out(transistor_17_out), .gate(_2));
  Transistor #(.\type ("n")) transistor_85 (.in(1'b0), .out(transistor_18_out), .gate(_2));
  Transistor #(.\type ("n")) transistor_86 (.in(1'b0), .out(transistor_18_out), .gate(_1));
  Transistor #(.\type ("n")) transistor_87 (.in(1'b0), .out(transistor_9_out), .gate(_2));
  Transistor #(.\type ("n")) transistor_88 (.in(1'b0), .out(transistor_9_out), .gate(_1));
  Transistor #(.\type ("n")) transistor_89 (.in(1'b0), .out(transistor_10_out), .gate(_1));
  Transistor #(.\type ("n")) transistor_90 (.in(1'b0), .out(transistor_10_out), .gate(_2));
  Transistor #(.\type ("n")) transistor_91 (.in(1'b0), .out(transistor_1_out), .gate(_0));
  Transistor #(.\type ("n")) transistor_92 (.in(1'b0), .out(transistor_12_out), .gate(_0));
  Transistor #(.\type ("n")) transistor_93 (.in(1'b0), .out(transistor_3_out), .gate(_0));
  Transistor #(.\type ("n")) transistor_94 (.in(1'b0), .out(transistor_7_out), .gate(_0));
  Transistor #(.\type ("n")) transistor_95 (.in(1'b0), .out(transistor_17_out), .gate(_0));
  Transistor #(.\type ("n")) transistor_96 (.in(1'b0), .out(transistor_18_out), .gate(_0));
  Transistor #(.\type ("n")) transistor_97 (.in(1'b0), .out(transistor_10_out), .gate(_0));
  Pull_Resistor #(.pull(1)) pull_resistor_1 (.node(transistor_1_out));
  Pull_Resistor #(.pull(1)) pull_resistor_2 (.node(transistor_12_out));
  Pull_Resistor #(.pull(1)) pull_resistor_3 (.node(transistor_34_out));
  Pull_Resistor #(.pull(1)) pull_resistor_4 (.node(transistor_2_out));
  Pull_Resistor #(.pull(1)) pull_resistor_5 (.node(transistor_3_out));
  Pull_Resistor #(.pull(1)) pull_resistor_6 (.node(transistor_15_out));
  Pull_Resistor #(.pull(1)) pull_resistor_7 (.node(transistor_5_out));
  Pull_Resistor #(.pull(1)) pull_resistor_8 (.node(transistor_7_out));
  Pull_Resistor #(.pull(1)) pull_resistor_9 (.node(transistor_17_out));
  Pull_Resistor #(.pull(1)) pull_resistor_10 (.node(transistor_18_out));
  Pull_Resistor #(.pull(1)) pull_resistor_11 (.node(transistor_9_out));
  Pull_Resistor #(.pull(1)) pull_resistor_12 (.node(transistor_10_out));
endmodule

module SEL_16x12_G (
  input  PCLK,
  input  _15,
  input  _14,
  input  _13,
  input  _12,
  input  _11,
  input  _10,
  input  _9,
  input  _8,
  input  _7,
  input  _6,
  input  _5,
  input  _4,
  input  _3,
  input  _2,
  input  _1,
  input  _0,
  output OUT0,
  output OUT1,
  output OUT2,
  output OUT3,
  output OUT4,
  output OUT5,
  output OUT6,
  output OUT7,
  output OUT8,
  output OUT9,
  output OUT10,
  output OUT11
);

  wire not_1_out, transistor_1_out, transistor_2_out, transistor_3_out, transistor_4_out, transistor_5_out,
       transistor_7_out, transistor_8_out, transistor_9_out, transistor_15_out, transistor_16_out,
       transistor_21_out, transistor_26_out;

  not not_1 (not_1_out, PCLK);
  and and_1 (OUT0, not_1_out, transistor_1_out);
  and and_2 (OUT1, not_1_out, transistor_2_out);
  and and_3 (OUT2, not_1_out, transistor_26_out);
  and and_4 (OUT3, not_1_out, transistor_3_out);
  and and_5 (OUT4, not_1_out, transistor_4_out);
  and and_6 (OUT5, not_1_out, transistor_15_out);
  and and_7 (OUT6, not_1_out, transistor_16_out);
  and and_8 (OUT7, not_1_out, transistor_5_out);
  and and_9 (OUT8, not_1_out, transistor_7_out);
  and and_10 (OUT9, not_1_out, transistor_21_out);
  and and_11 (OUT10, not_1_out, transistor_8_out);
  and and_12 (OUT11, not_1_out, transistor_9_out);
  Transistor #(.\type ("n")) transistor_1 (.in(1'b0), .out(transistor_1_out), .gate(_14));
  Transistor #(.\type ("n")) transistor_2 (.in(1'b0), .out(transistor_2_out), .gate(_15));
  Transistor #(.\type ("n")) transistor_3 (.in(1'b0), .out(transistor_3_out), .gate(_15));
  Transistor #(.\type ("n")) transistor_4 (.in(1'b0), .out(transistor_4_out), .gate(_15));
  Transistor #(.\type ("n")) transistor_5 (.in(1'b0), .out(transistor_5_out), .gate(_14));
  Transistor #(.\type ("n")) transistor_6 (.in(1'b0), .out(transistor_5_out), .gate(_15));
  Transistor #(.\type ("n")) transistor_7 (.in(1'b0), .out(transistor_7_out), .gate(_14));
  Transistor #(.\type ("n")) transistor_8 (.in(1'b0), .out(transistor_8_out), .gate(_14));
  Transistor #(.\type ("n")) transistor_9 (.in(1'b0), .out(transistor_9_out), .gate(_14));
  Transistor #(.\type ("n")) transistor_10 (.in(1'b0), .out(transistor_9_out), .gate(_15));
  Transistor #(.\type ("n")) transistor_11 (.in(1'b0), .out(transistor_1_out), .gate(_13));
  Transistor #(.\type ("n")) transistor_12 (.in(1'b0), .out(transistor_2_out), .gate(_13));
  Transistor #(.\type ("n")) transistor_13 (.in(1'b0), .out(transistor_3_out), .gate(_12));
  Transistor #(.\type ("n")) transistor_14 (.in(1'b0), .out(transistor_3_out), .gate(_13));
  Transistor #(.\type ("n")) transistor_15 (.in(1'b0), .out(transistor_15_out), .gate(_13));
  Transistor #(.\type ("n")) transistor_16 (.in(1'b0), .out(transistor_16_out), .gate(_12));
  Transistor #(.\type ("n")) transistor_17 (.in(1'b0), .out(transistor_5_out), .gate(_13));
  Transistor #(.\type ("n")) transistor_18 (.in(1'b0), .out(transistor_5_out), .gate(_12));
  Transistor #(.\type ("n")) transistor_19 (.in(1'b0), .out(transistor_7_out), .gate(_13));
  Transistor #(.\type ("n")) transistor_20 (.in(1'b0), .out(transistor_7_out), .gate(_12));
  Transistor #(.\type ("n")) transistor_21 (.in(1'b0), .out(transistor_21_out), .gate(_12));
  Transistor #(.\type ("n")) transistor_22 (.in(1'b0), .out(transistor_21_out), .gate(_13));
  Transistor #(.\type ("n")) transistor_23 (.in(1'b0), .out(transistor_8_out), .gate(_13));
  Transistor #(.\type ("n")) transistor_24 (.in(1'b0), .out(transistor_9_out), .gate(_12));
  Transistor #(.\type ("n")) transistor_25 (.in(1'b0), .out(transistor_1_out), .gate(_11));
  Transistor #(.\type ("n")) transistor_26 (.in(1'b0), .out(transistor_26_out), .gate(_11));
  Transistor #(.\type ("n")) transistor_27 (.in(1'b0), .out(transistor_15_out), .gate(_11));
  Transistor #(.\type ("n")) transistor_28 (.in(1'b0), .out(transistor_16_out), .gate(_11));
  Transistor #(.\type ("n")) transistor_29 (.in(1'b0), .out(transistor_5_out), .gate(_11));
  Transistor #(.\type ("n")) transistor_30 (.in(1'b0), .out(transistor_7_out), .gate(_11));
  Transistor #(.\type ("n")) transistor_31 (.in(1'b0), .out(transistor_21_out), .gate(_11));
  Transistor #(.\type ("n")) transistor_32 (.in(1'b0), .out(transistor_8_out), .gate(_11));
  Transistor #(.\type ("n")) transistor_33 (.in(1'b0), .out(transistor_9_out), .gate(_11));
  Transistor #(.\type ("n")) transistor_34 (.in(1'b0), .out(transistor_1_out), .gate(_9));
  Transistor #(.\type ("n")) transistor_35 (.in(1'b0), .out(transistor_2_out), .gate(_10));
  Transistor #(.\type ("n")) transistor_36 (.in(1'b0), .out(transistor_2_out), .gate(_9));
  Transistor #(.\type ("n")) transistor_37 (.in(1'b0), .out(transistor_26_out), .gate(_10));
  Transistor #(.\type ("n")) transistor_38 (.in(1'b0), .out(transistor_26_out), .gate(_9));
  Transistor #(.\type ("n")) transistor_39 (.in(1'b0), .out(transistor_3_out), .gate(_9));
  Transistor #(.\type ("n")) transistor_40 (.in(1'b0), .out(transistor_4_out), .gate(_10));
  Transistor #(.\type ("n")) transistor_41 (.in(1'b0), .out(transistor_4_out), .gate(_9));
  Transistor #(.\type ("n")) transistor_42 (.in(1'b0), .out(transistor_16_out), .gate(_9));
  Transistor #(.\type ("n")) transistor_43 (.in(1'b0), .out(transistor_5_out), .gate(_10));
  Transistor #(.\type ("n")) transistor_44 (.in(1'b0), .out(transistor_7_out), .gate(_9));
  Transistor #(.\type ("n")) transistor_45 (.in(1'b0), .out(transistor_21_out), .gate(_9));
  Transistor #(.\type ("n")) transistor_46 (.in(1'b0), .out(transistor_8_out), .gate(_9));
  Transistor #(.\type ("n")) transistor_47 (.in(1'b0), .out(transistor_9_out), .gate(_10));
  Transistor #(.\type ("n")) transistor_48 (.in(1'b0), .out(transistor_2_out), .gate(_8));
  Transistor #(.\type ("n")) transistor_49 (.in(1'b0), .out(transistor_3_out), .gate(_8));
  Transistor #(.\type ("n")) transistor_50 (.in(1'b0), .out(transistor_4_out), .gate(_8));
  Transistor #(.\type ("n")) transistor_51 (.in(1'b0), .out(transistor_15_out), .gate(_8));
  Transistor #(.\type ("n")) transistor_52 (.in(1'b0), .out(transistor_16_out), .gate(_8));
  Transistor #(.\type ("n")) transistor_53 (.in(1'b0), .out(transistor_5_out), .gate(_8));
  Transistor #(.\type ("n")) transistor_54 (.in(1'b0), .out(transistor_8_out), .gate(_8));
  Transistor #(.\type ("n")) transistor_55 (.in(1'b0), .out(transistor_9_out), .gate(_8));
  Transistor #(.\type ("n")) transistor_56 (.in(1'b0), .out(transistor_2_out), .gate(_7));
  Transistor #(.\type ("n")) transistor_57 (.in(1'b0), .out(transistor_26_out), .gate(_7));
  Transistor #(.\type ("n")) transistor_58 (.in(1'b0), .out(transistor_3_out), .gate(_7));
  Transistor #(.\type ("n")) transistor_59 (.in(1'b0), .out(transistor_3_out), .gate(_6));
  Transistor #(.\type ("n")) transistor_60 (.in(1'b0), .out(transistor_15_out), .gate(_6));
  Transistor #(.\type ("n")) transistor_61 (.in(1'b0), .out(transistor_16_out), .gate(_7));
  Transistor #(.\type ("n")) transistor_62 (.in(1'b0), .out(transistor_16_out), .gate(_6));
  Transistor #(.\type ("n")) transistor_63 (.in(1'b0), .out(transistor_5_out), .gate(_6));
  Transistor #(.\type ("n")) transistor_64 (.in(1'b0), .out(transistor_21_out), .gate(_7));
  Transistor #(.\type ("n")) transistor_65 (.in(1'b0), .out(transistor_8_out), .gate(_7));
  Transistor #(.\type ("n")) transistor_66 (.in(1'b0), .out(transistor_8_out), .gate(_6));
  Transistor #(.\type ("n")) transistor_67 (.in(1'b0), .out(transistor_1_out), .gate(_5));
  Transistor #(.\type ("n")) transistor_68 (.in(1'b0), .out(transistor_1_out), .gate(_4));
  Transistor #(.\type ("n")) transistor_69 (.in(1'b0), .out(transistor_2_out), .gate(_5));
  Transistor #(.\type ("n")) transistor_70 (.in(1'b0), .out(transistor_26_out), .gate(_4));
  Transistor #(.\type ("n")) transistor_71 (.in(1'b0), .out(transistor_3_out), .gate(_4));
  Transistor #(.\type ("n")) transistor_72 (.in(1'b0), .out(transistor_4_out), .gate(_4));
  Transistor #(.\type ("n")) transistor_73 (.in(1'b0), .out(transistor_4_out), .gate(_5));
  Transistor #(.\type ("n")) transistor_74 (.in(1'b0), .out(transistor_15_out), .gate(_5));
  Transistor #(.\type ("n")) transistor_75 (.in(1'b0), .out(transistor_15_out), .gate(_4));
  Transistor #(.\type ("n")) transistor_76 (.in(1'b0), .out(transistor_16_out), .gate(_5));
  Transistor #(.\type ("n")) transistor_77 (.in(1'b0), .out(transistor_16_out), .gate(_4));
  Transistor #(.\type ("n")) transistor_78 (.in(1'b0), .out(transistor_7_out), .gate(_5));
  Transistor #(.\type ("n")) transistor_79 (.in(1'b0), .out(transistor_21_out), .gate(_5));
  Transistor #(.\type ("n")) transistor_80 (.in(1'b0), .out(transistor_21_out), .gate(_4));
  Transistor #(.\type ("n")) transistor_81 (.in(1'b0), .out(transistor_8_out), .gate(_4));
  Transistor #(.\type ("n")) transistor_82 (.in(1'b0), .out(transistor_9_out), .gate(_5));
  Transistor #(.\type ("n")) transistor_83 (.in(1'b0), .out(transistor_2_out), .gate(_3));
  Transistor #(.\type ("n")) transistor_84 (.in(1'b0), .out(transistor_4_out), .gate(_3));
  Transistor #(.\type ("n")) transistor_85 (.in(1'b0), .out(transistor_15_out), .gate(_3));
  Transistor #(.\type ("n")) transistor_86 (.in(1'b0), .out(transistor_21_out), .gate(_3));
  Transistor #(.\type ("n")) transistor_87 (.in(1'b0), .out(transistor_1_out), .gate(_2));
  Transistor #(.\type ("n")) transistor_88 (.in(1'b0), .out(transistor_2_out), .gate(_1));
  Transistor #(.\type ("n")) transistor_89 (.in(1'b0), .out(transistor_3_out), .gate(_2));
  Transistor #(.\type ("n")) transistor_90 (.in(1'b0), .out(transistor_3_out), .gate(_1));
  Transistor #(.\type ("n")) transistor_91 (.in(1'b0), .out(transistor_15_out), .gate(_1));
  Transistor #(.\type ("n")) transistor_92 (.in(1'b0), .out(transistor_16_out), .gate(_1));
  Transistor #(.\type ("n")) transistor_93 (.in(1'b0), .out(transistor_7_out), .gate(_2));
  Transistor #(.\type ("n")) transistor_94 (.in(1'b0), .out(transistor_21_out), .gate(_1));
  Transistor #(.\type ("n")) transistor_95 (.in(1'b0), .out(transistor_8_out), .gate(_2));
  Transistor #(.\type ("n")) transistor_96 (.in(1'b0), .out(transistor_9_out), .gate(_2));
  Transistor #(.\type ("n")) transistor_97 (.in(1'b0), .out(transistor_1_out), .gate(_0));
  Transistor #(.\type ("n")) transistor_98 (.in(1'b0), .out(transistor_3_out), .gate(_0));
  Transistor #(.\type ("n")) transistor_99 (.in(1'b0), .out(transistor_5_out), .gate(_0));
  Transistor #(.\type ("n")) transistor_100 (.in(1'b0), .out(transistor_7_out), .gate(_0));
  Transistor #(.\type ("n")) transistor_101 (.in(1'b0), .out(transistor_8_out), .gate(_0));
  Transistor #(.\type ("n")) transistor_102 (.in(1'b0), .out(transistor_9_out), .gate(_0));
  Pull_Resistor #(.pull(1)) pull_resistor_1 (.node(transistor_1_out));
  Pull_Resistor #(.pull(1)) pull_resistor_2 (.node(transistor_2_out));
  Pull_Resistor #(.pull(1)) pull_resistor_3 (.node(transistor_26_out));
  Pull_Resistor #(.pull(1)) pull_resistor_4 (.node(transistor_3_out));
  Pull_Resistor #(.pull(1)) pull_resistor_5 (.node(transistor_4_out));
  Pull_Resistor #(.pull(1)) pull_resistor_6 (.node(transistor_15_out));
  Pull_Resistor #(.pull(1)) pull_resistor_7 (.node(transistor_16_out));
  Pull_Resistor #(.pull(1)) pull_resistor_8 (.node(transistor_5_out));
  Pull_Resistor #(.pull(1)) pull_resistor_9 (.node(transistor_7_out));
  Pull_Resistor #(.pull(1)) pull_resistor_10 (.node(transistor_21_out));
  Pull_Resistor #(.pull(1)) pull_resistor_11 (.node(transistor_8_out));
  Pull_Resistor #(.pull(1)) pull_resistor_12 (.node(transistor_9_out));
endmodule

module SEL_16x12_B (
  input  PCLK,
  input  _15,
  input  _14,
  input  _13,
  input  _12,
  input  _11,
  input  _10,
  input  _9,
  input  _8,
  input  _7,
  input  _6,
  input  _5,
  input  _4,
  input  _3,
  input  _2,
  input  _1,
  input  _0,
  output OUT0,
  output OUT1,
  output OUT2,
  output OUT3,
  output OUT4,
  output OUT5,
  output OUT6,
  output OUT7,
  output OUT8,
  output OUT9,
  output OUT10,
  output OUT11
);

  wire not_1_out, transistor_1_out, transistor_2_out, transistor_3_out, transistor_4_out, transistor_6_out,
       transistor_7_out, transistor_8_out, transistor_10_out, transistor_13_out, transistor_14_out,
       transistor_18_out, transistor_20_out;

  not not_1 (not_1_out, PCLK);
  and and_1 (OUT0, not_1_out, transistor_1_out);
  and and_2 (OUT1, not_1_out, transistor_10_out);
  and and_3 (OUT2, not_1_out, transistor_2_out);
  and and_4 (OUT3, not_1_out, transistor_3_out);
  and and_5 (OUT4, not_1_out, transistor_4_out);
  and and_6 (OUT5, not_1_out, transistor_13_out);
  and and_7 (OUT6, not_1_out, transistor_14_out);
  and and_8 (OUT7, not_1_out, transistor_6_out);
  and and_9 (OUT8, not_1_out, transistor_7_out);
  and and_10 (OUT9, not_1_out, transistor_18_out);
  and and_11 (OUT10, not_1_out, transistor_20_out);
  and and_12 (OUT11, not_1_out, transistor_8_out);
  Transistor #(.\type ("n")) transistor_1 (.in(1'b0), .out(transistor_1_out), .gate(_14));
  Transistor #(.\type ("n")) transistor_2 (.in(1'b0), .out(transistor_2_out), .gate(_15));
  Transistor #(.\type ("n")) transistor_3 (.in(1'b0), .out(transistor_3_out), .gate(_14));
  Transistor #(.\type ("n")) transistor_4 (.in(1'b0), .out(transistor_4_out), .gate(_15));
  Transistor #(.\type ("n")) transistor_5 (.in(1'b0), .out(transistor_4_out), .gate(_14));
  Transistor #(.\type ("n")) transistor_6 (.in(1'b0), .out(transistor_6_out), .gate(_14));
  Transistor #(.\type ("n")) transistor_7 (.in(1'b0), .out(transistor_7_out), .gate(_14));
  Transistor #(.\type ("n")) transistor_8 (.in(1'b0), .out(transistor_8_out), .gate(_14));
  Transistor #(.\type ("n")) transistor_9 (.in(1'b0), .out(transistor_1_out), .gate(_13));
  Transistor #(.\type ("n")) transistor_10 (.in(1'b0), .out(transistor_10_out), .gate(_13));
  Transistor #(.\type ("n")) transistor_11 (.in(1'b0), .out(transistor_2_out), .gate(_12));
  Transistor #(.\type ("n")) transistor_12 (.in(1'b0), .out(transistor_4_out), .gate(_13));
  Transistor #(.\type ("n")) transistor_13 (.in(1'b0), .out(transistor_13_out), .gate(_13));
  Transistor #(.\type ("n")) transistor_14 (.in(1'b0), .out(transistor_14_out), .gate(_13));
  Transistor #(.\type ("n")) transistor_15 (.in(1'b0), .out(transistor_6_out), .gate(_12));
  Transistor #(.\type ("n")) transistor_16 (.in(1'b0), .out(transistor_6_out), .gate(_13));
  Transistor #(.\type ("n")) transistor_17 (.in(1'b0), .out(transistor_7_out), .gate(_13));
  Transistor #(.\type ("n")) transistor_18 (.in(1'b0), .out(transistor_18_out), .gate(_12));
  Transistor #(.\type ("n")) transistor_19 (.in(1'b0), .out(transistor_18_out), .gate(_13));
  Transistor #(.\type ("n")) transistor_20 (.in(1'b0), .out(transistor_20_out), .gate(_13));
  Transistor #(.\type ("n")) transistor_21 (.in(1'b0), .out(transistor_8_out), .gate(_13));
  Transistor #(.\type ("n")) transistor_22 (.in(1'b0), .out(transistor_8_out), .gate(_12));
  Transistor #(.\type ("n")) transistor_23 (.in(1'b0), .out(transistor_2_out), .gate(_11));
  Transistor #(.\type ("n")) transistor_24 (.in(1'b0), .out(transistor_13_out), .gate(_11));
  Transistor #(.\type ("n")) transistor_25 (.in(1'b0), .out(transistor_18_out), .gate(_11));
  Transistor #(.\type ("n")) transistor_26 (.in(1'b0), .out(transistor_1_out), .gate(_10));
  Transistor #(.\type ("n")) transistor_27 (.in(1'b0), .out(transistor_10_out), .gate(_10));
  Transistor #(.\type ("n")) transistor_28 (.in(1'b0), .out(transistor_2_out), .gate(_9));
  Transistor #(.\type ("n")) transistor_29 (.in(1'b0), .out(transistor_2_out), .gate(_10));
  Transistor #(.\type ("n")) transistor_30 (.in(1'b0), .out(transistor_3_out), .gate(_9));
  Transistor #(.\type ("n")) transistor_31 (.in(1'b0), .out(transistor_3_out), .gate(_10));
  Transistor #(.\type ("n")) transistor_32 (.in(1'b0), .out(transistor_13_out), .gate(_10));
  Transistor #(.\type ("n")) transistor_33 (.in(1'b0), .out(transistor_14_out), .gate(_10));
  Transistor #(.\type ("n")) transistor_34 (.in(1'b0), .out(transistor_14_out), .gate(_9));
  Transistor #(.\type ("n")) transistor_35 (.in(1'b0), .out(transistor_6_out), .gate(_10));
  Transistor #(.\type ("n")) transistor_36 (.in(1'b0), .out(transistor_7_out), .gate(_9));
  Transistor #(.\type ("n")) transistor_37 (.in(1'b0), .out(transistor_18_out), .gate(_9));
  Transistor #(.\type ("n")) transistor_38 (.in(1'b0), .out(transistor_18_out), .gate(_10));
  Transistor #(.\type ("n")) transistor_39 (.in(1'b0), .out(transistor_20_out), .gate(_9));
  Transistor #(.\type ("n")) transistor_40 (.in(1'b0), .out(transistor_20_out), .gate(_10));
  Transistor #(.\type ("n")) transistor_41 (.in(1'b0), .out(transistor_8_out), .gate(_10));
  Transistor #(.\type ("n")) transistor_42 (.in(1'b0), .out(transistor_10_out), .gate(_8));
  Transistor #(.\type ("n")) transistor_43 (.in(1'b0), .out(transistor_3_out), .gate(_8));
  Transistor #(.\type ("n")) transistor_44 (.in(1'b0), .out(transistor_4_out), .gate(_8));
  Transistor #(.\type ("n")) transistor_45 (.in(1'b0), .out(transistor_13_out), .gate(_8));
  Transistor #(.\type ("n")) transistor_46 (.in(1'b0), .out(transistor_6_out), .gate(_8));
  Transistor #(.\type ("n")) transistor_47 (.in(1'b0), .out(transistor_18_out), .gate(_8));
  Transistor #(.\type ("n")) transistor_48 (.in(1'b0), .out(transistor_8_out), .gate(_8));
  Transistor #(.\type ("n")) transistor_49 (.in(1'b0), .out(transistor_1_out), .gate(_7));
  Transistor #(.\type ("n")) transistor_50 (.in(1'b0), .out(transistor_10_out), .gate(_6));
  Transistor #(.\type ("n")) transistor_51 (.in(1'b0), .out(transistor_10_out), .gate(_7));
  Transistor #(.\type ("n")) transistor_52 (.in(1'b0), .out(transistor_2_out), .gate(_6));
  Transistor #(.\type ("n")) transistor_53 (.in(1'b0), .out(transistor_2_out), .gate(_7));
  Transistor #(.\type ("n")) transistor_54 (.in(1'b0), .out(transistor_3_out), .gate(_6));
  Transistor #(.\type ("n")) transistor_55 (.in(1'b0), .out(transistor_4_out), .gate(_7));
  Transistor #(.\type ("n")) transistor_56 (.in(1'b0), .out(transistor_13_out), .gate(_7));
  Transistor #(.\type ("n")) transistor_57 (.in(1'b0), .out(transistor_13_out), .gate(_6));
  Transistor #(.\type ("n")) transistor_58 (.in(1'b0), .out(transistor_14_out), .gate(_6));
  Transistor #(.\type ("n")) transistor_59 (.in(1'b0), .out(transistor_6_out), .gate(_6));
  Transistor #(.\type ("n")) transistor_60 (.in(1'b0), .out(transistor_7_out), .gate(_7));
  Transistor #(.\type ("n")) transistor_61 (.in(1'b0), .out(transistor_18_out), .gate(_6));
  Transistor #(.\type ("n")) transistor_62 (.in(1'b0), .out(transistor_20_out), .gate(_6));
  Transistor #(.\type ("n")) transistor_63 (.in(1'b0), .out(transistor_1_out), .gate(_4));
  Transistor #(.\type ("n")) transistor_64 (.in(1'b0), .out(transistor_10_out), .gate(_5));
  Transistor #(.\type ("n")) transistor_65 (.in(1'b0), .out(transistor_2_out), .gate(_4));
  Transistor #(.\type ("n")) transistor_66 (.in(1'b0), .out(transistor_3_out), .gate(_5));
  Transistor #(.\type ("n")) transistor_67 (.in(1'b0), .out(transistor_4_out), .gate(_4));
  Transistor #(.\type ("n")) transistor_68 (.in(1'b0), .out(transistor_13_out), .gate(_4));
  Transistor #(.\type ("n")) transistor_69 (.in(1'b0), .out(transistor_14_out), .gate(_4));
  Transistor #(.\type ("n")) transistor_70 (.in(1'b0), .out(transistor_6_out), .gate(_5));
  Transistor #(.\type ("n")) transistor_71 (.in(1'b0), .out(transistor_7_out), .gate(_4));
  Transistor #(.\type ("n")) transistor_72 (.in(1'b0), .out(transistor_18_out), .gate(_4));
  Transistor #(.\type ("n")) transistor_73 (.in(1'b0), .out(transistor_20_out), .gate(_4));
  Transistor #(.\type ("n")) transistor_74 (.in(1'b0), .out(transistor_8_out), .gate(_4));
  Transistor #(.\type ("n")) transistor_75 (.in(1'b0), .out(transistor_8_out), .gate(_5));
  Transistor #(.\type ("n")) transistor_76 (.in(1'b0), .out(transistor_10_out), .gate(_3));
  Transistor #(.\type ("n")) transistor_77 (.in(1'b0), .out(transistor_2_out), .gate(_3));
  Transistor #(.\type ("n")) transistor_78 (.in(1'b0), .out(transistor_13_out), .gate(_3));
  Transistor #(.\type ("n")) transistor_79 (.in(1'b0), .out(transistor_18_out), .gate(_3));
  Transistor #(.\type ("n")) transistor_80 (.in(1'b0), .out(transistor_20_out), .gate(_3));
  Transistor #(.\type ("n")) transistor_81 (.in(1'b0), .out(transistor_1_out), .gate(_2));
  Transistor #(.\type ("n")) transistor_82 (.in(1'b0), .out(transistor_1_out), .gate(_1));
  Transistor #(.\type ("n")) transistor_83 (.in(1'b0), .out(transistor_10_out), .gate(_2));
  Transistor #(.\type ("n")) transistor_84 (.in(1'b0), .out(transistor_10_out), .gate(_1));
  Transistor #(.\type ("n")) transistor_85 (.in(1'b0), .out(transistor_2_out), .gate(_2));
  Transistor #(.\type ("n")) transistor_86 (.in(1'b0), .out(transistor_3_out), .gate(_2));
  Transistor #(.\type ("n")) transistor_87 (.in(1'b0), .out(transistor_3_out), .gate(_1));
  Transistor #(.\type ("n")) transistor_88 (.in(1'b0), .out(transistor_13_out), .gate(_2));
  Transistor #(.\type ("n")) transistor_89 (.in(1'b0), .out(transistor_13_out), .gate(_1));
  Transistor #(.\type ("n")) transistor_90 (.in(1'b0), .out(transistor_14_out), .gate(_2));
  Transistor #(.\type ("n")) transistor_91 (.in(1'b0), .out(transistor_6_out), .gate(_1));
  Transistor #(.\type ("n")) transistor_92 (.in(1'b0), .out(transistor_6_out), .gate(_2));
  Transistor #(.\type ("n")) transistor_93 (.in(1'b0), .out(transistor_7_out), .gate(_2));
  Transistor #(.\type ("n")) transistor_94 (.in(1'b0), .out(transistor_18_out), .gate(_1));
  Transistor #(.\type ("n")) transistor_95 (.in(1'b0), .out(transistor_18_out), .gate(_2));
  Transistor #(.\type ("n")) transistor_96 (.in(1'b0), .out(transistor_20_out), .gate(_2));
  Transistor #(.\type ("n")) transistor_97 (.in(1'b0), .out(transistor_8_out), .gate(_2));
  Transistor #(.\type ("n")) transistor_98 (.in(1'b0), .out(transistor_1_out), .gate(_0));
  Transistor #(.\type ("n")) transistor_99 (.in(1'b0), .out(transistor_2_out), .gate(_0));
  Transistor #(.\type ("n")) transistor_100 (.in(1'b0), .out(transistor_14_out), .gate(_0));
  Transistor #(.\type ("n")) transistor_101 (.in(1'b0), .out(transistor_7_out), .gate(_0));
  Transistor #(.\type ("n")) transistor_102 (.in(1'b0), .out(transistor_18_out), .gate(_0));
  Transistor #(.\type ("n")) transistor_103 (.in(1'b0), .out(transistor_20_out), .gate(_0));
  Pull_Resistor #(.pull(1)) pull_resistor_1 (.node(transistor_1_out));
  Pull_Resistor #(.pull(1)) pull_resistor_2 (.node(transistor_10_out));
  Pull_Resistor #(.pull(1)) pull_resistor_3 (.node(transistor_2_out));
  Pull_Resistor #(.pull(1)) pull_resistor_4 (.node(transistor_3_out));
  Pull_Resistor #(.pull(1)) pull_resistor_5 (.node(transistor_4_out));
  Pull_Resistor #(.pull(1)) pull_resistor_6 (.node(transistor_13_out));
  Pull_Resistor #(.pull(1)) pull_resistor_7 (.node(transistor_14_out));
  Pull_Resistor #(.pull(1)) pull_resistor_8 (.node(transistor_6_out));
  Pull_Resistor #(.pull(1)) pull_resistor_9 (.node(transistor_7_out));
  Pull_Resistor #(.pull(1)) pull_resistor_10 (.node(transistor_18_out));
  Pull_Resistor #(.pull(1)) pull_resistor_11 (.node(transistor_20_out));
  Pull_Resistor #(.pull(1)) pull_resistor_12 (.node(transistor_8_out));
endmodule

module SEL4x16 (
  input  PCLK,
  input  L0,
  input  L1,
  input  C2,
  input  C3,
  output _15,
  output _14,
  output _13,
  output _12,
  output _11,
  output _10,
  output _9,
  output _8,
  output _7,
  output _6,
  output _5,
  output _4,
  output _3,
  output _2,
  output _1,
  output _0
);

  wire not_1_out, not_2_out, not_3_out, not_4_out, not_5_out, transistor_1_out, transistor_5_out,
       transistor_9_out, transistor_13_out, transistor_17_out, transistor_18_out, transistor_25_out,
       transistor_29_out, transistor_33_out, transistor_37_out, transistor_41_out, transistor_45_out,
       transistor_49_out, transistor_50_out, transistor_57_out, transistor_61_out;

  not not_1 (not_1_out, PCLK);
  not not_2 (not_2_out, L0);
  not not_3 (not_3_out, L1);
  not not_4 (not_4_out, C2);
  not not_5 (not_5_out, C3);
  and and_1 (_15, not_1_out, transistor_1_out);
  Transistor #(.\type ("n")) transistor_1 (.in(1'b0), .out(transistor_1_out), .gate(not_2_out));
  Transistor #(.\type ("n")) transistor_2 (.in(1'b0), .out(transistor_1_out), .gate(not_3_out));
  Transistor #(.\type ("n")) transistor_3 (.in(1'b0), .out(transistor_1_out), .gate(not_4_out));
  Transistor #(.\type ("n")) transistor_4 (.in(1'b0), .out(transistor_1_out), .gate(not_5_out));
  Pull_Resistor #(.pull(1)) pull_resistor_1 (.node(transistor_1_out));
  and and_2 (_14, not_1_out, transistor_5_out);
  Transistor #(.\type ("n")) transistor_5 (.in(1'b0), .out(transistor_5_out), .gate(not_2_out));
  Transistor #(.\type ("n")) transistor_6 (.in(1'b0), .out(transistor_5_out), .gate(not_3_out));
  Transistor #(.\type ("n")) transistor_7 (.in(1'b0), .out(transistor_5_out), .gate(C2));
  Transistor #(.\type ("n")) transistor_8 (.in(1'b0), .out(transistor_5_out), .gate(not_5_out));
  Pull_Resistor #(.pull(1)) pull_resistor_2 (.node(transistor_5_out));
  and and_3 (_13, not_1_out, transistor_9_out);
  Transistor #(.\type ("n")) transistor_9 (.in(1'b0), .out(transistor_9_out), .gate(not_2_out));
  Transistor #(.\type ("n")) transistor_10 (.in(1'b0), .out(transistor_9_out), .gate(not_3_out));
  Transistor #(.\type ("n")) transistor_11 (.in(1'b0), .out(transistor_9_out), .gate(not_4_out));
  Transistor #(.\type ("n")) transistor_12 (.in(1'b0), .out(transistor_9_out), .gate(C3));
  Pull_Resistor #(.pull(1)) pull_resistor_3 (.node(transistor_9_out));
  and and_4 (_11, not_1_out, transistor_17_out);
  and and_5 (_12, not_1_out, transistor_13_out);
  Transistor #(.\type ("n")) transistor_13 (.in(1'b0), .out(transistor_13_out), .gate(not_2_out));
  Transistor #(.\type ("n")) transistor_14 (.in(1'b0), .out(transistor_13_out), .gate(not_3_out));
  Transistor #(.\type ("n")) transistor_15 (.in(1'b0), .out(transistor_13_out), .gate(C2));
  Transistor #(.\type ("n")) transistor_16 (.in(1'b0), .out(transistor_13_out), .gate(C3));
  Pull_Resistor #(.pull(1)) pull_resistor_4 (.node(transistor_13_out));
  and and_6 (_10, not_1_out, transistor_18_out);
  Transistor #(.\type ("n")) transistor_17 (.in(1'b0), .out(transistor_17_out), .gate(L0));
  Transistor #(.\type ("n")) transistor_18 (.in(1'b0), .out(transistor_18_out), .gate(L0));
  Transistor #(.\type ("n")) transistor_19 (.in(1'b0), .out(transistor_17_out), .gate(not_3_out));
  Transistor #(.\type ("n")) transistor_20 (.in(1'b0), .out(transistor_18_out), .gate(not_3_out));
  Transistor #(.\type ("n")) transistor_21 (.in(1'b0), .out(transistor_18_out), .gate(C2));
  Transistor #(.\type ("n")) transistor_22 (.in(1'b0), .out(transistor_17_out), .gate(not_4_out));
  Transistor #(.\type ("n")) transistor_23 (.in(1'b0), .out(transistor_18_out), .gate(not_5_out));
  Transistor #(.\type ("n")) transistor_24 (.in(1'b0), .out(transistor_17_out), .gate(not_5_out));
  Pull_Resistor #(.pull(1)) pull_resistor_5 (.node(transistor_18_out));
  Pull_Resistor #(.pull(1)) pull_resistor_6 (.node(transistor_17_out));
  and and_7 (_9, not_1_out, transistor_25_out);
  Transistor #(.\type ("n")) transistor_25 (.in(1'b0), .out(transistor_25_out), .gate(L0));
  Transistor #(.\type ("n")) transistor_26 (.in(1'b0), .out(transistor_25_out), .gate(not_3_out));
  Transistor #(.\type ("n")) transistor_27 (.in(1'b0), .out(transistor_25_out), .gate(not_4_out));
  Transistor #(.\type ("n")) transistor_28 (.in(1'b0), .out(transistor_25_out), .gate(C3));
  Pull_Resistor #(.pull(1)) pull_resistor_7 (.node(transistor_25_out));
  and and_8 (_8, not_1_out, transistor_29_out);
  Transistor #(.\type ("n")) transistor_29 (.in(1'b0), .out(transistor_29_out), .gate(L0));
  Transistor #(.\type ("n")) transistor_30 (.in(1'b0), .out(transistor_29_out), .gate(not_3_out));
  Transistor #(.\type ("n")) transistor_31 (.in(1'b0), .out(transistor_29_out), .gate(C2));
  Transistor #(.\type ("n")) transistor_32 (.in(1'b0), .out(transistor_29_out), .gate(C3));
  Pull_Resistor #(.pull(1)) pull_resistor_8 (.node(transistor_29_out));
  and and_9 (_7, not_1_out, transistor_33_out);
  Transistor #(.\type ("n")) transistor_33 (.in(1'b0), .out(transistor_33_out), .gate(not_2_out));
  Transistor #(.\type ("n")) transistor_34 (.in(1'b0), .out(transistor_33_out), .gate(L1));
  Transistor #(.\type ("n")) transistor_35 (.in(1'b0), .out(transistor_33_out), .gate(not_4_out));
  Transistor #(.\type ("n")) transistor_36 (.in(1'b0), .out(transistor_33_out), .gate(not_5_out));
  Pull_Resistor #(.pull(1)) pull_resistor_9 (.node(transistor_33_out));
  and and_10 (_6, not_1_out, transistor_37_out);
  Transistor #(.\type ("n")) transistor_37 (.in(1'b0), .out(transistor_37_out), .gate(not_2_out));
  Transistor #(.\type ("n")) transistor_38 (.in(1'b0), .out(transistor_37_out), .gate(L1));
  Transistor #(.\type ("n")) transistor_39 (.in(1'b0), .out(transistor_37_out), .gate(C2));
  Transistor #(.\type ("n")) transistor_40 (.in(1'b0), .out(transistor_37_out), .gate(not_5_out));
  Pull_Resistor #(.pull(1)) pull_resistor_10 (.node(transistor_37_out));
  and and_11 (_5, not_1_out, transistor_41_out);
  Transistor #(.\type ("n")) transistor_41 (.in(1'b0), .out(transistor_41_out), .gate(not_2_out));
  Transistor #(.\type ("n")) transistor_42 (.in(1'b0), .out(transistor_41_out), .gate(L1));
  Transistor #(.\type ("n")) transistor_43 (.in(1'b0), .out(transistor_41_out), .gate(not_4_out));
  Transistor #(.\type ("n")) transistor_44 (.in(1'b0), .out(transistor_41_out), .gate(C3));
  Pull_Resistor #(.pull(1)) pull_resistor_11 (.node(transistor_41_out));
  and and_12 (_3, not_1_out, transistor_50_out);
  and and_13 (_4, not_1_out, transistor_45_out);
  Transistor #(.\type ("n")) transistor_45 (.in(1'b0), .out(transistor_45_out), .gate(not_2_out));
  Transistor #(.\type ("n")) transistor_46 (.in(1'b0), .out(transistor_45_out), .gate(L1));
  Transistor #(.\type ("n")) transistor_47 (.in(1'b0), .out(transistor_45_out), .gate(C2));
  Transistor #(.\type ("n")) transistor_48 (.in(1'b0), .out(transistor_45_out), .gate(C3));
  Pull_Resistor #(.pull(1)) pull_resistor_12 (.node(transistor_45_out));
  and and_14 (_2, not_1_out, transistor_49_out);
  Transistor #(.\type ("n")) transistor_49 (.in(1'b0), .out(transistor_49_out), .gate(L0));
  Transistor #(.\type ("n")) transistor_50 (.in(1'b0), .out(transistor_50_out), .gate(L0));
  Transistor #(.\type ("n")) transistor_51 (.in(1'b0), .out(transistor_50_out), .gate(L1));
  Transistor #(.\type ("n")) transistor_52 (.in(1'b0), .out(transistor_49_out), .gate(L1));
  Transistor #(.\type ("n")) transistor_53 (.in(1'b0), .out(transistor_49_out), .gate(C2));
  Transistor #(.\type ("n")) transistor_54 (.in(1'b0), .out(transistor_50_out), .gate(not_4_out));
  Transistor #(.\type ("n")) transistor_55 (.in(1'b0), .out(transistor_50_out), .gate(not_5_out));
  Transistor #(.\type ("n")) transistor_56 (.in(1'b0), .out(transistor_49_out), .gate(not_5_out));
  Pull_Resistor #(.pull(1)) pull_resistor_13 (.node(transistor_50_out));
  Pull_Resistor #(.pull(1)) pull_resistor_14 (.node(transistor_49_out));
  and and_15 (_1, not_1_out, transistor_57_out);
  Transistor #(.\type ("n")) transistor_57 (.in(1'b0), .out(transistor_57_out), .gate(L0));
  Transistor #(.\type ("n")) transistor_58 (.in(1'b0), .out(transistor_57_out), .gate(L1));
  Transistor #(.\type ("n")) transistor_59 (.in(1'b0), .out(transistor_57_out), .gate(not_4_out));
  Transistor #(.\type ("n")) transistor_60 (.in(1'b0), .out(transistor_57_out), .gate(C3));
  Pull_Resistor #(.pull(1)) pull_resistor_15 (.node(transistor_57_out));
  and and_16 (_0, not_1_out, transistor_61_out);
  Transistor #(.\type ("n")) transistor_61 (.in(1'b0), .out(transistor_61_out), .gate(L0));
  Transistor #(.\type ("n")) transistor_62 (.in(1'b0), .out(transistor_61_out), .gate(L1));
  Transistor #(.\type ("n")) transistor_63 (.in(1'b0), .out(transistor_61_out), .gate(C2));
  Transistor #(.\type ("n")) transistor_64 (.in(1'b0), .out(transistor_61_out), .gate(C3));
  Pull_Resistor #(.pull(1)) pull_resistor_16 (.node(transistor_61_out));
endmodule
