// Logisim project 2C07_PPU_PAL.circ as structural Verilog: 50 circuits, main circuit 2C07_PPU
// PIX_SELECT
module _2C07_PPU (
  input  nDBE,
  input  RS2,
  input  RS1,
  input  RS0,
  input  R_W,
  input  D7,
  input  D6,
  input  D5,
  input  D4,
  input  D3,
  input  D2,
  input  D1,
  input  D0,
  input  PD0,
  input  PD1,
  input  PD2,
  input  PD3,
  input  PD4,
  input  PD5,
  input  PD6,
  input  PD7,
  input  nRES,
  input  in_23,
  input  in_24,
  input  in_25,
  input  in_26,
  input  in_27,
  input  in_28,
  input  in_29,
  input  in_30,
  input  EXT3,
  input  EXT2,
  input  EXT1,
  input  EXT0,
  output D7_2,
  output D6_2,
  output D5_2,
  output D4_2,
  output D3_2,
  output D2_2,
  output D1_2,
  output D0_2,
  output ALE,
  output nWR,
  output nRD,
  output PA13,
  output PA12,
  output PA11,
  output PA10,
  output PA9,
  output PA8,
  output PA7,
  output PA6,
  output PA5,
  output PA4,
  output PA3,
  output PA2,
  output PA1,
  output PA0,
  output PD0_W,
  output PD1_W,
  output PD2_W,
  output PD3_W,
  output PD4_W,
  output PD5_W,
  output PD6_W,
  output PD7_W,
  output nINT,
  output [10:0] VOUT,
  output out_70,
  output out_71,
  output out_72,
  output out_73
);

  wire bg_color_1_bgc0, bg_color_1_bgc1, bg_color_1_bgc2, bg_color_1_bgc3, BLNK, CLK_out,
       color_control_1_cb_db, color_control_1_color_en, color_control_1_db_cb, color_io_1_cb_ram0,
       color_io_1_cb_ram1, color_io_1_cb_ram2, color_io_1_cb_ram3, color_io_1_cb_ram4, color_io_1_cb_ram5,
       color_io_1_nout0, color_io_1_nout1, color_io_1_nout2, color_io_1_nout3, color_io_1_nout4,
       color_io_1_nout5, color_ram_1_ram_cb0, color_ram_1_ram_cb1, color_ram_1_ram_cb2, color_ram_1_ram_cb3,
       color_ram_1_ram_cy0, color_ram_1_ram_cy1, control_regs_1_bgsel, control_regs_1_black,
       control_regs_1_bw, control_regs_1_clpb, control_regs_1_clpo, control_regs_1_i1_32,
       control_regs_1_nbgclip, control_regs_1_nobclip, control_regs_1_nslave, control_regs_1_o8_16,
       control_regs_1_obsel, control_regs_1_vbl, control_unit_1__0_hpos, control_unit_1_burst,
       control_unit_1_clip_b, control_unit_1_clip_o, control_unit_1_e_ev, control_unit_1_eval,
       control_unit_1_f_at, control_unit_1_f_nt, control_unit_1_f_ta, control_unit_1_f_tb, control_unit_1_hc,
       control_unit_1_nfo, control_unit_1_picture, control_unit_1_s_ev, control_unit_1_sc_cnt,
       control_unit_1_sync, control_unit_1_unk_pal_oam_ctrl, control_unit_1_vb, control_unit_1_vc,
       control_unit_1_vin, controlled_buffer_1_out, DB5, DB6, DB7, DB_PAR, H0_prime, H0_prime_prime,
       H1_prime, H2_prime, h_counter_1_h0, h_counter_1_h1, h_counter_1_h2, h_counter_1_h3, h_counter_1_h4,
       h_counter_1_h5, h_counter_1_h6, h_counter_1_h7, h_counter_1_h8, hv_select_1__0, hv_select_1__0_1,
       hv_select_1__0_7__256_263, hv_select_1__0_63, hv_select_1__0_255, hv_select_1__0_255_2,
       hv_select_1__0___255, hv_select_1__1, hv_select_1__2_3, hv_select_1__4, hv_select_1__4_5,
       hv_select_1__6_7, hv_select_1__63, hv_select_1__65, hv_select_1__240, hv_select_1__240_2,
       hv_select_1__241, hv_select_1__255, hv_select_1__256, hv_select_1__256_2, hv_select_1__256_319,
       hv_select_1__265, hv_select_1__269, hv_select_1__272, hv_select_1__277, hv_select_1__277_2,
       hv_select_1__302, hv_select_1__306, hv_select_1__311, hv_select_1__311_2, hv_select_1__320_355,
       hv_select_1__321, hv_select_1__339, hv_select_1__340, I_OAM2, interrupt_control_1_int, nR2, nR7, nVIS,
       oam_buf_control_1_db_ob, oam_buf_control_1_noe, oam_buf_control_1_ofetch, oam_buffer_bit_1_or,
       oam_buffer_bit_1_ow, oam_control_1_milf, oam_control_1_wtf, oam_eval_1__0_fifo, oam_eval_1_lol,
       oam_eval_1_omfg, oam_fifo_1_spr0hit, PAR_O, PCLK, picture_address_gen_1_tvo1, RC,
       register_select_1_nr4, register_select_1_nw0, register_select_1_nw1, register_select_1_nw3,
       register_select_1_nw4, register_select_1_nw5_1, register_select_1_nw5_2, register_select_1_nw6_1,
       register_select_1_nw6_2, register_select_1_nw7, RES, RESCL, rw_control_1_nrd, rw_control_1_nwr,
       select_each_2_3_5_7_pix_1_sh2, select_each_2_3_5_7_pix_1_sh3, select_each_2_3_5_7_pix_1_sh5,
       select_each_2_3_5_7_pix_1_sh7, TH_MUX, v_counter_1_v0, v_counter_1_v1, v_counter_1_v2, v_counter_1_v3,
       v_counter_1_v4, v_counter_1_v5, v_counter_1_v6, v_counter_1_v7, v_counter_1_v8, VCLR,
       vram_bus_control_1_pd_rb, vram_bus_control_1_tstep, vram_bus_control_1_xrb;
  wire [2:0] control_regs_1_ntr, picture_address_gen_1_fh0;
  wire [3:0] oam_eval_1_ov0;
  wire [4:0] mux_1_pal0, oam_fifo_1_zcol0, TH;
  wire [5:0] hv_select_1_hnn;
  wire [5:1] Hnn_BUS;
  wire [7:0] color_io_1_db0_2, cpu_data_pad_8_cpu_ppu, h_inversion_1_t0, hv_select_1_vpos;

  Clock CLK (.out(CLK_out));
  not not_1 (nINT, interrupt_control_1_int);
  assign controlled_buffer_1_out = nRES ? PCLK : 1'bz;  // Controlled_Buffer controlled_buffer_1
  COLOR_IO color_io_1 (
    .PCLK(PCLK), .CB_DB(color_control_1_cb_db), .DB0_2(color_io_1_db0_2[0]), .RAM_CB0(color_ram_1_ram_cb0),
    .nout0(color_io_1_nout0), .DB_CB(color_control_1_db_cb), .DB0(cpu_data_pad_8_cpu_ppu[0]),
    .CB_RAM0(color_io_1_cb_ram0), .DB1_2(color_io_1_db0_2[1]), .nout1(color_io_1_nout1),
    .DB2_2(color_io_1_db0_2[2]), .nout2(color_io_1_nout2), .DB3_2(color_io_1_db0_2[3]),
    .nout3(color_io_1_nout3), .DB4_2(DB5), .nout4(color_io_1_nout4), .DB5_2(DB6), .nout5(color_io_1_nout5),
    .nBW(color_control_1_color_en), .DB1(cpu_data_pad_8_cpu_ppu[1]), .CB_RAM1(color_io_1_cb_ram1),
    .DB2(cpu_data_pad_8_cpu_ppu[2]), .CB_RAM2(color_io_1_cb_ram2), .DB3(cpu_data_pad_8_cpu_ppu[3]),
    .CB_RAM3(color_io_1_cb_ram3), .DB4(cpu_data_pad_8_cpu_ppu[4]), .CB_RAM4(color_io_1_cb_ram4),
    .DB5(cpu_data_pad_8_cpu_ppu[5]), .CB_RAM5(color_io_1_cb_ram5), .RAM_CB5(color_ram_1_ram_cy1),
    .RAM_CB4(color_ram_1_ram_cy0), .RAM_CB3(color_ram_1_ram_cb3), .RAM_CB2(color_ram_1_ram_cb2),
    .RAM_CB1(color_ram_1_ram_cb1));
  OAM_CONTROL oam_control_1 (
    .PCLK(controlled_buffer_1_out), .DB0(cpu_data_pad_8_cpu_ppu[0]), .DB1(cpu_data_pad_8_cpu_ppu[1]),
    .DB2(cpu_data_pad_8_cpu_ppu[2]), .DB3(cpu_data_pad_8_cpu_ppu[3]), .DB4(cpu_data_pad_8_cpu_ppu[4]),
    .DB5(cpu_data_pad_8_cpu_ppu[5]), .DB6(cpu_data_pad_8_cpu_ppu[6]), .DB7(cpu_data_pad_8_cpu_ppu[7]),
    .nDBE(nDBE), .nW3(register_select_1_nw3), .I_OAM2(I_OAM2), .nVIS(nVIS), .H0_prime_prime(H0_prime_prime),
    .BLNK(BLNK), .OFETCH(oam_buf_control_1_ofetch), .EVAL(control_unit_1_eval), .RESCL(RESCL), .nR2(nR2),
    .DB5_2(DB5), .H0_prime(H0_prime), .MILF(oam_control_1_milf), .PAR_O(PAR_O), .H2_prime(H2_prime),
    .OMFG(oam_eval_1_omfg), .WTF(oam_control_1_wtf));  // open: nOAM0, nOAM1, nOAM2, nOAM3, nOAM4, nOAM5, nOAM6, nOAM7, nOAM8
  OAM_BUFFER_BIT oam_buffer_bit_1 (
    .PCLK(PCLK), .IOAM2(I_OAM2), .nR4(register_select_1_nr4), .OB___DB(DB5), .DB_OB(oam_buf_control_1_db_ob),
    .nOE(oam_buf_control_1_noe), .OR(oam_buffer_bit_1_or), .OW(oam_buffer_bit_1_ow),
    .DB___OB(cpu_data_pad_8_cpu_ppu[7]));  // open: OB
  PIXEL_CLOCK pixel_clock_1 (.CLK(CLK_out), .RES(RES), .PCLK(PCLK));
  RESET_FF reset_ff_1 (.nRES(nRES), .RESCL(VCLR), .RES(RES), .RC(RC));
  VIDEO_OUT video_out_1 (
    .CLK(CLK_out), .RES(RES), .nTR(control_regs_1_ntr[0]), .nTG(control_regs_1_ntr[1]),
    .nTB(control_regs_1_ntr[2]), .PCLK(PCLK), .nCC0(color_io_1_nout0), .nCC1(color_io_1_nout1),
    .nCC2(color_io_1_nout2), .nCC3(color_io_1_nout3), .SYNC(control_unit_1_sync),
    .BURST(control_unit_1_burst), .PICTURE(control_unit_1_picture), .nLL0(color_io_1_nout5),
    .nLL1(color_io_1_nout4), .out_17(VOUT), .V0(v_counter_1_v0));
  COLOR_RAM color_ram_1 (
    .PAL2(mux_1_pal0[2]), .PAL3(mux_1_pal0[1]), .PCLK(PCLK), .PAL4(mux_1_pal0[0]), .PAL0(mux_1_pal0[4]),
    .PAL1(mux_1_pal0[3]), .CB3_RAM(color_io_1_cb_ram3), .RAM_CB3(color_ram_1_ram_cb3),
    .CB2_RAM(color_io_1_cb_ram2), .RAM_CB2(color_ram_1_ram_cb2), .CB1_RAM(color_io_1_cb_ram1),
    .RAM_CB1(color_ram_1_ram_cb1), .CB0_RAM(color_io_1_cb_ram0), .RAM_CB0(color_ram_1_ram_cb0),
    .CY1_RAM(color_io_1_cb_ram5), .RAM_CY1(color_ram_1_ram_cy1), .CY0_RAM(color_io_1_cb_ram4),
    .RAM_CY0(color_ram_1_ram_cy0));
  INTERRUPT_CONTROL interrupt_control_1 (
    .VSET(RESCL), .VCLR(VCLR), .nDBE(nDBE), .nR2(nR2), .VBL_EN(control_regs_1_vbl),
    .INT(interrupt_control_1_int), .DB7(DB7));
  COLOR_CONTROL color_control_1 (
    .PCLK(PCLK), .DB_PAR(DB_PAR), .PICTURE(control_unit_1_picture), .BW(control_regs_1_bw), .TH_MUX(TH_MUX),
    .nR7(nR7), .nDBE(nDBE), .DB_CB(color_control_1_db_cb), .CB_DB(color_control_1_cb_db),
    .COLOR_EN(color_control_1_color_en));
  OAM_EVAL oam_eval_1 (
    .PCLK(PCLK), .H0_prime_prime(H0_prime_prime), .I_OAM2(I_OAM2), .F_NT(control_unit_1_f_nt),
    .S_EV(control_unit_1_s_ev), .PAR_O(PAR_O), .V0(hv_select_1_vpos[0]), .V1(hv_select_1_vpos[1]),
    .V2(hv_select_1_vpos[2]), .V3(hv_select_1_vpos[3]), .V4(hv_select_1_vpos[4]), .V5(hv_select_1_vpos[5]),
    .V6(hv_select_1_vpos[6]), .V7(hv_select_1_vpos[7]), .OB0(in_23), .OB1(in_24), .OB2(in_25), .OB3(in_26),
    .OB4(in_27), .OB5(in_28), .OB6(in_29), .OB7(in_30), .OV0(oam_eval_1_ov0[0]), .OV1(oam_eval_1_ov0[1]),
    .OV2(oam_eval_1_ov0[2]), .OV3(oam_eval_1_ov0[3]), .O8_16(control_regs_1_o8_16), .OMFG(oam_eval_1_omfg),
    .nVIS(nVIS), .WTF(oam_control_1_wtf), ._0_FIFO(oam_eval_1__0_fifo), .LOL(oam_eval_1_lol));
  OAM_BUF_CONTROL oam_buf_control_1 (
    .PCLK(PCLK), .BLNK(BLNK), .WTF(oam_control_1_wtf), .nVIS(nVIS), .MILF(oam_control_1_milf),
    .H0_prime_prime(H0_prime_prime), .nW4(register_select_1_nw4), .nDBE(nDBE),
    .DB_OB(oam_buf_control_1_db_ob), .nOE(oam_buf_control_1_noe), .OFETCH(oam_buf_control_1_ofetch));
  HV_SELECT hv_select_1 (
    .H8(h_counter_1_h8), .H7(h_counter_1_h7), .H6(h_counter_1_h6), .H5(h_counter_1_h5), .H4(h_counter_1_h4),
    .H3(h_counter_1_h3), .H2(h_counter_1_h2), .H1(h_counter_1_h1), .H0(h_counter_1_h0),
    .VB(control_unit_1_vb), .BLNK(BLNK), ._277(hv_select_1__277), ._256(hv_select_1__256),
    ._65(hv_select_1__65), ._0_7__256_263(hv_select_1__0_7__256_263), ._0_255(hv_select_1__0_255),
    ._339(hv_select_1__339), ._63(hv_select_1__63), ._255(hv_select_1__255), ._0_63(hv_select_1__0_63),
    ._256_319(hv_select_1__256_319), ._0_255_2(hv_select_1__0_255_2), ._0_1(hv_select_1__0_1),
    ._6_7(hv_select_1__6_7), ._4_5(hv_select_1__4_5), ._320_355(hv_select_1__320_355),
    ._0___255(hv_select_1__0___255), ._2_3(hv_select_1__2_3), ._256_2(hv_select_1__256_2),
    ._4(hv_select_1__4), ._277_2(hv_select_1__277_2), ._302(hv_select_1__302), ._321(hv_select_1__321),
    ._306(hv_select_1__306), ._340(hv_select_1__340), ._272(hv_select_1__272), .V8(v_counter_1_v8),
    .V7(v_counter_1_v7), .V6(v_counter_1_v6), .V5(v_counter_1_v5), .V4(v_counter_1_v4), .V3(v_counter_1_v3),
    .V2(v_counter_1_v2), .V1(v_counter_1_v1), .V0(v_counter_1_v0), ._269(hv_select_1__269),
    ._240(hv_select_1__240), ._241(hv_select_1__241), ._0(hv_select_1__0), ._240_2(hv_select_1__240_2),
    ._311_2(hv_select_1__311_2), .Hnn(hv_select_1_hnn), .VPOS(hv_select_1_vpos), ._265(hv_select_1__265),
    ._311(hv_select_1__311), ._1(hv_select_1__1));
  H_COUNTER h_counter_1 (
    .HC(control_unit_1_hc), .RES(RES), .CLK(PCLK), .H0(h_counter_1_h0), .H1(h_counter_1_h1),
    .H2(h_counter_1_h2), .H3(h_counter_1_h3), .H4(h_counter_1_h4), .H5(h_counter_1_h5), .H6(h_counter_1_h6),
    .H7(h_counter_1_h7), .H8(h_counter_1_h8));
  SELECT_EACH_2_3_5_7_PIX select_each_2_3_5_7_pix_1 (
    .PCLK(PCLK), .SH2(select_each_2_3_5_7_pix_1_sh2), .H0_prime_prime(H0_prime_prime),
    .H1_prime_prime(Hnn_BUS[1]), .H2_prime_prime(Hnn_BUS[2]), .PAR_O(PAR_O),
    .SH3(select_each_2_3_5_7_pix_1_sh3), .SH5(select_each_2_3_5_7_pix_1_sh5),
    .SH7(select_each_2_3_5_7_pix_1_sh7));
  V_COUNTER v_counter_1 (
    .VC(control_unit_1_vc), .RES(RES), .CLK(PCLK), .V0(v_counter_1_v0), .V1(v_counter_1_v1),
    .V2(v_counter_1_v2), .V3(v_counter_1_v3), .V4(v_counter_1_v4), .V5(v_counter_1_v5), .V6(v_counter_1_v6),
    .V7(v_counter_1_v7), .V8(v_counter_1_v8), .VIN(control_unit_1_vin));
  H_INVERSION h_inversion_1 (
    .OB6(in_29), .PCLK(PCLK), .PD0(PD0), .PD1(PD1), .PD2(PD2), .PD3(PD3), .PD4(PD4), .PD5(PD5), .PD6(PD6),
    .PD7(PD7), .T0(h_inversion_1_t0[0]), .T1(h_inversion_1_t0[1]), .T2(h_inversion_1_t0[2]),
    .T3(h_inversion_1_t0[3]), .T4(h_inversion_1_t0[4]), .T5(h_inversion_1_t0[5]), .T6(h_inversion_1_t0[6]),
    .T7(h_inversion_1_t0[7]), .SH2(select_each_2_3_5_7_pix_1_sh2), ._0_FIFO(oam_eval_1__0_fifo));
  CONTROL_UNIT control_unit_1 (
    .PCLK(PCLK), .nOBCLIP(control_regs_1_nobclip), .nBGCLIP(control_regs_1_nbgclip), .BLACK(1'b0),
    ._277_2(hv_select_1__277), ._256(hv_select_1__256), ._65(hv_select_1__65),
    ._0_7__256_263(hv_select_1__0_7__256_263), ._0_255(hv_select_1__0_255), ._339(hv_select_1__339),
    ._63(hv_select_1__63), ._255(hv_select_1__255), ._0_63(hv_select_1__0_63),
    ._256_319(hv_select_1__256_319), ._0_255_2(hv_select_1__0_255_2), ._0_1(hv_select_1__0_1),
    ._6_7(hv_select_1__6_7), ._4_5(hv_select_1__4_5), ._320_355(hv_select_1__320_355),
    ._0_255_3(hv_select_1__0___255), ._2_3(hv_select_1__2_3), ._4(hv_select_1__4), ._277(hv_select_1__277_2),
    ._302(hv_select_1__302), ._321(hv_select_1__321), ._306(hv_select_1__306), ._272(hv_select_1__272),
    ._269(hv_select_1__269), ._1(hv_select_1__1), ._240(hv_select_1__240), ._241(hv_select_1__241),
    ._0(hv_select_1__0), ._240_2(hv_select_1__240_2), ._311(hv_select_1__311), ._311_2(hv_select_1__311_2),
    .S_EV(control_unit_1_s_ev), .CLIP_O(control_unit_1_clip_o), .CLIP_B(control_unit_1_clip_b),
    ._0_HPOS(control_unit_1__0_hpos), .EVAL(control_unit_1_eval), .E_EV(control_unit_1_e_ev),
    .I_OAM2(I_OAM2), .PAR_O(PAR_O), .nVIS(nVIS), .F_NT(control_unit_1_f_nt), .F_TB(control_unit_1_f_tb),
    .F_TA(control_unit_1_f_ta), .nFO(control_unit_1_nfo), .F_AT(control_unit_1_f_at),
    .SC_CNT(control_unit_1_sc_cnt), .SYNC(control_unit_1_sync), .BURST(control_unit_1_burst),
    .PICTURE(control_unit_1_picture), .VSET(RESCL), .VB(control_unit_1_vb), .BLNK(BLNK), .VCLR(VCLR),
    ._340(hv_select_1__340), .VIN(control_unit_1_vin), .HC(control_unit_1_hc), .VC(control_unit_1_vc),
    .Hnn(hv_select_1_hnn), .H0_prime_prime(H0_prime_prime), .H1_prime_prime(Hnn_BUS[1]),
    .H2_prime_prime(Hnn_BUS[2]), .H3_prime_prime(Hnn_BUS[3]), .H4_prime_prime(Hnn_BUS[4]),
    .H5_prime_prime(Hnn_BUS[5]), .H0_prime(H0_prime), .H1_prime(H1_prime), .H2_prime(H2_prime),
    ._256_2(hv_select_1__256_2), ._265(hv_select_1__265), .UNK_PAL_OAM_CTRL(control_unit_1_unk_pal_oam_ctrl));
  OAM_FIFO oam_fifo_1 (
    .PCLK(PCLK), .SH2(select_each_2_3_5_7_pix_1_sh2), .nVIS(nVIS), .SH5(select_each_2_3_5_7_pix_1_sh5),
    .SH7(select_each_2_3_5_7_pix_1_sh7), .H5_prime_prime(Hnn_BUS[5]), .H4_prime_prime(Hnn_BUS[4]),
    .H3_prime_prime(Hnn_BUS[3]), .SH3(select_each_2_3_5_7_pix_1_sh3), .CLPO(control_regs_1_clpo),
    .ZCOL0(oam_fifo_1_zcol0[0]), .ZCOL1(oam_fifo_1_zcol0[1]), .ZCOL2(oam_fifo_1_zcol0[2]),
    .ZCOL3(oam_fifo_1_zcol0[3]), .ZPRIO(oam_fifo_1_zcol0[4]), .OB0(in_23), .OB1(in_24), .OB2(in_25),
    .OB3(in_26), .OB4(in_27), .OB5(in_28), .OB6(in_29), .OB7(in_30), .T0(h_inversion_1_t0[0]),
    .T1(h_inversion_1_t0[1]), .T2(h_inversion_1_t0[2]), .T3(h_inversion_1_t0[3]), .T4(h_inversion_1_t0[4]),
    .T5(h_inversion_1_t0[5]), .T6(h_inversion_1_t0[6]), .T7(h_inversion_1_t0[7]),
    .SPR0HIT(oam_fifo_1_spr0hit), ._0_HPOS(control_unit_1__0_hpos));
  CONTROL_REGS control_regs_1 (
    .nDBE(nDBE), .nW0(register_select_1_nw0), .RC(RC), .nW1(register_select_1_nw1),
    .DB0(cpu_data_pad_8_cpu_ppu[0]), .DB1(cpu_data_pad_8_cpu_ppu[1]), .DB2(cpu_data_pad_8_cpu_ppu[2]),
    .DB3(cpu_data_pad_8_cpu_ppu[3]), .DB4(cpu_data_pad_8_cpu_ppu[4]), .DB5(cpu_data_pad_8_cpu_ppu[5]),
    .DB6(cpu_data_pad_8_cpu_ppu[6]), .DB7(cpu_data_pad_8_cpu_ppu[7]), .BW(control_regs_1_bw),
    .I1_32(control_regs_1_i1_32), .OBSEL(control_regs_1_obsel), .nBGCLIP(control_regs_1_nbgclip),
    .BGSEL(control_regs_1_bgsel), .nOBCLIP(control_regs_1_nobclip), .CLPB(control_regs_1_clpb),
    .BLACK(control_regs_1_black), .O8_16(control_regs_1_o8_16), .nSLAVE(control_regs_1_nslave),
    .CLPO(control_regs_1_clpo), .VBL(control_regs_1_vbl), .nTR(control_regs_1_ntr[0]),
    .nTG(control_regs_1_ntr[1]), .nTB(control_regs_1_ntr[2]), .PCLK(PCLK), .CLIP_B(control_unit_1_clip_b),
    .CLIP_O(control_unit_1_clip_o), .nVIS(nVIS));
  RW_CONTROL rw_control_1 (.R_W(R_W), .nDBE(nDBE), .nRD(rw_control_1_nrd), .nWR(rw_control_1_nwr));
  REGISTER_SELECT register_select_1 (
    .nDBE(nDBE), .RC(RC), .RS0(RS0), .RS1(RS1), .RS2(RS2), .R_W(R_W), .nW6_1(register_select_1_nw6_1),
    .nW6_2(register_select_1_nw6_2), .nW5_1(register_select_1_nw5_1), .nW5_2(register_select_1_nw5_2),
    .nR7(nR7), .nW7(register_select_1_nw7), .nW4(register_select_1_nw4), .nW3(register_select_1_nw3),
    .nR2(nR2), .nW1(register_select_1_nw1), .nW0(register_select_1_nw0), .nR4(register_select_1_nr4));
  CPU_DATA_PAD cpu_data_pad_1 (
    .nRD(rw_control_1_nrd), .nWR(rw_control_1_nwr), .PPU_CPU(color_io_1_db0_2[7]),
    .CPU_PPU(cpu_data_pad_8_cpu_ppu[7]), .PPU_ADRESS_OUT(D7_2), .PPU_data_in(D7));
  CPU_DATA_PAD cpu_data_pad_2 (
    .nRD(rw_control_1_nrd), .nWR(rw_control_1_nwr), .PPU_CPU(DB7), .CPU_PPU(cpu_data_pad_8_cpu_ppu[6]),
    .PPU_ADRESS_OUT(D6_2), .PPU_data_in(D6));
  CPU_DATA_PAD cpu_data_pad_3 (
    .nRD(rw_control_1_nrd), .nWR(rw_control_1_nwr), .PPU_CPU(DB6), .CPU_PPU(cpu_data_pad_8_cpu_ppu[5]),
    .PPU_ADRESS_OUT(D5_2), .PPU_data_in(D5));
  CPU_DATA_PAD cpu_data_pad_4 (
    .nRD(rw_control_1_nrd), .nWR(rw_control_1_nwr), .PPU_CPU(DB5), .CPU_PPU(cpu_data_pad_8_cpu_ppu[4]),
    .PPU_ADRESS_OUT(D4_2), .PPU_data_in(D4));
  CPU_DATA_PAD cpu_data_pad_5 (
    .nRD(rw_control_1_nrd), .nWR(rw_control_1_nwr), .PPU_CPU(color_io_1_db0_2[3]),
    .CPU_PPU(cpu_data_pad_8_cpu_ppu[3]), .PPU_ADRESS_OUT(D3_2), .PPU_data_in(D3));
  VRAM_BUS_CONTROL vram_bus_control_1 (
    .PCLK(PCLK), .H0_prime(H0_prime), .BLNK(BLNK), .nR7(nR7), .nW7(register_select_1_nw7), .nDBE(nDBE),
    .nPA8(PA8), .nPA9(PA9), .nPA10(PA10), .nPA11(PA11), .nPA12(PA12), .WR(nWR),
    .PD_RB(vram_bus_control_1_pd_rb), .nALE(ALE), .TSTEP(vram_bus_control_1_tstep), .DB_PAR(DB_PAR),
    .RD(nRD), .TH_MUX(TH_MUX), .XRB(vram_bus_control_1_xrb), .RES(RES));
  PICTURE_ADDRESS_GEN picture_address_gen_1 (
    .PCLK(PCLK), .DB0(cpu_data_pad_8_cpu_ppu[0]), .nDBE(nDBE), .RC(RC), .nW5_1(register_select_1_nw6_2),
    .DB1(cpu_data_pad_8_cpu_ppu[1]), .DB2(cpu_data_pad_8_cpu_ppu[2]), .PD0(PD0), .PD1(PD1), .PD2(PD2),
    .PD3(PD3), .PD4(PD4), .PD5(PD5), .PD6(PD6), .PD7(PD7), .DB3(cpu_data_pad_8_cpu_ppu[3]),
    .DB4(cpu_data_pad_8_cpu_ppu[4]), .DB5(cpu_data_pad_8_cpu_ppu[5]), .DB6(cpu_data_pad_8_cpu_ppu[6]),
    .DB7(cpu_data_pad_8_cpu_ppu[7]), .nW0(register_select_1_nw0), .nW6_2(register_select_1_nw5_1),
    .nW5_2(register_select_1_nw5_2), .nW6_1(register_select_1_nw6_1), .FH0(picture_address_gen_1_fh0[0]),
    .FH1(picture_address_gen_1_fh0[1]), .FH2(picture_address_gen_1_fh0[2]), .BLNK(BLNK),
    .l1_32(control_regs_1_i1_32), .TSTEP(vram_bus_control_1_tstep), .E_EV(control_unit_1_e_ev),
    .F_TB(control_unit_1_f_tb), .F_AT(control_unit_1_f_at), .H2_prime(H2_prime), .PA11(PA11), .PA10(PA10),
    .PA12(PA12), .PA9(PA9), .PA8(PA8), .PA7(PA7), .PA6(PA6), .PA5(PA5), .PA4(PA4), .PA3(PA3), .PA2(PA2),
    .PA1(PA1), .PA0(PA0), .OB0(in_23), .OB1(in_24), .OB2(in_25), .OB3(in_26), .OB4(in_27), .OB5(in_28),
    .OB6(in_29), .OB7(in_30), .THO1(TH[1]), .THO2(TH[2]), .THO3(TH[3]), .THO4(TH[4]), .RESCL(VCLR),
    .SC_CNT(control_unit_1_sc_cnt), .PAR_O(PAR_O), .F_NT(control_unit_1_f_nt), .BGSEL(control_regs_1_bgsel),
    .O8_16(control_regs_1_o8_16), .OBSEL(control_regs_1_obsel), .OV0(oam_eval_1_ov0[0]),
    .OV1(oam_eval_1_ov0[1]), .OV2(oam_eval_1_ov0[2]), .OV3(oam_eval_1_ov0[3]), .H1_prime(H1_prime),
    .SH2(select_each_2_3_5_7_pix_1_sh2), .H0_prime_prime(H0_prime_prime), .TVO1(picture_address_gen_1_tvo1),
    .THO0(TH[0]), .PA13(PA13));
  BG_COLOR bg_color_1 (
    .PCLK(PCLK), .PD0(PD0), .PD1(PD1), .PD2(PD2), .PD3(PD3), .PD4(PD4), .PD5(PD5), .PD6(PD6), .PD7(PD7),
    .CLPB(control_regs_1_clpb), .F_TA(control_unit_1_f_ta), .F_TB(control_unit_1_f_tb),
    .F_AT(control_unit_1_f_at), .nFO(control_unit_1_nfo), .H0_prime_prime(H0_prime_prime), .THO1(TH[1]),
    .TVO1(picture_address_gen_1_tvo1), .FH0(picture_address_gen_1_fh0[0]),
    .FH1(picture_address_gen_1_fh0[1]), .FH2(picture_address_gen_1_fh0[2]), .BGC0(bg_color_1_bgc0),
    .BGC1(bg_color_1_bgc1), .BGC2(bg_color_1_bgc2), .BGC3(bg_color_1_bgc3));
  MUX mux_1 (
    .PCLK(PCLK), .BGC0(bg_color_1_bgc0), .BGC1(bg_color_1_bgc1), .BGC2(bg_color_1_bgc2),
    .BGC3(bg_color_1_bgc3), .ZCOL0(oam_fifo_1_zcol0[0]), .ZCOL1(oam_fifo_1_zcol0[1]),
    .ZCOL2(oam_fifo_1_zcol0[2]), .ZCOL3(oam_fifo_1_zcol0[3]), .ZPRIO(oam_fifo_1_zcol0[4]), .EXT0_IN(EXT0),
    .EXT1_IN(EXT1), .EXT2_IN(EXT2), .EXT3_IN(EXT3), .THO0(TH[0]), .THO1(TH[1]), .THO2(TH[2]), .THO3(TH[3]),
    .THO4(TH[4]), .TH_MUX(TH_MUX), .PAL0(mux_1_pal0[0]), .PAL1(mux_1_pal0[1]), .PAL2(mux_1_pal0[2]),
    .PAL3(mux_1_pal0[3]), .PAL4(mux_1_pal0[4]), .EXT0_OUT(out_73), .EXT1_OUT(out_72), .EXT2_OUT(out_71),
    .EXT3_OUT(out_70), .SPR0HIT(oam_fifo_1_spr0hit), .LOL(oam_eval_1_lol), .DB6(DB6), .nVIS(nVIS),
    .nDBE(nDBE), .nR2(nR2), .RESCL(RESCL));
  CPU_DATA_PAD cpu_data_pad_6 (
    .nRD(rw_control_1_nrd), .nWR(rw_control_1_nwr), .PPU_CPU(color_io_1_db0_2[2]),
    .CPU_PPU(cpu_data_pad_8_cpu_ppu[2]), .PPU_ADRESS_OUT(D2_2), .PPU_data_in(D2));
  CPU_DATA_PAD cpu_data_pad_7 (
    .nRD(rw_control_1_nrd), .nWR(rw_control_1_nwr), .PPU_CPU(color_io_1_db0_2[1]),
    .CPU_PPU(cpu_data_pad_8_cpu_ppu[1]), .PPU_ADRESS_OUT(D1_2), .PPU_data_in(D1));
  CPU_DATA_PAD cpu_data_pad_8 (
    .nRD(rw_control_1_nrd), .nWR(rw_control_1_nwr), .PPU_CPU(color_io_1_db0_2[0]),
    .CPU_PPU(cpu_data_pad_8_cpu_ppu[0]), .PPU_ADRESS_OUT(D0_2), .PPU_data_in(D0));
  READ__2007 read_2007_1 (
    .DB0(color_io_1_db0_2[0]), .XRB(vram_bus_control_1_xrb), .PD_RB(vram_bus_control_1_pd_rb), .PD0(PD0),
    .RC(RC), .DB1(color_io_1_db0_2[1]), .PD1(PD1), .DB2(color_io_1_db0_2[2]), .PD2(PD2),
    .DB3(color_io_1_db0_2[3]), .PD3(PD3), .DB4(DB5), .PD4(PD4), .DB5(DB6), .PD5(PD5), .DB6(DB7), .PD6(PD6),
    .DB7(color_io_1_db0_2[7]), .PD7(PD7));
  WRITE__2007 write_2007_1 (
    .PCLK(PCLK), .DB_PAR(DB_PAR), .D0(cpu_data_pad_8_cpu_ppu[0]), .D1(cpu_data_pad_8_cpu_ppu[1]),
    .D2(cpu_data_pad_8_cpu_ppu[2]), .D3(cpu_data_pad_8_cpu_ppu[3]), .D4(cpu_data_pad_8_cpu_ppu[4]),
    .D5(cpu_data_pad_8_cpu_ppu[5]), .D6(cpu_data_pad_8_cpu_ppu[6]), .D7(cpu_data_pad_8_cpu_ppu[7]),
    .PD0(PD0_W), .PD1(PD1_W), .PD2(PD2_W), .PD3(PD3_W), .PD4(PD4_W), .PD5(PD5_W), .PD6(PD6_W), .PD7(PD7_W));

  // Other names for the same wires on the sheet: Hnn_BUS[0] = H0_prime_prime;
  //   PPU_DATA[7:0] = {PD7, PD6, PD5, PD4, PD3, PD2, PD1, PD0};
  //   PPU_DATA_W[7:0] = {PD7_W, PD6_W, PD5_W, PD4_W, PD3_W, PD2_W, PD1_W, PD0_W}

  // Notes on the sheet:
  //   2C07 PPU
  //   UNK_PAL_OAM_CTRL
  //   CPU INTERFACE
  //   Logisim doesn't support bidirectional pads and wires
  //   So we have to add workaround by separate I/O wires
  //   MASTER/SLAVE
  //   VRAM INTERFACE
  //   Logisim doesn't support bidirectional pads and wires
  //   So we have to add workaround by separate I/O wires
endmodule

module D_latch (
  input  EN,
  input  D,
  output Q,
  output NOT_Q
);

  D_Flip_Flop #(.trigger("high")) d_ff_1 (.clk(EN), .D(D), .Q(Q), .Qn(NOT_Q));  // open: preset, en, reset
endmodule

module PIXEL_CLOCK (
  input  CLK,
  input  RES,
  output PCLK
);

  wire _2_out, _3_out, d_latch_1_q, d_latch_2_not_q, d_latch_3_not_q, d_latch_4_not_q, d_latch_5_not_q,
       d_latch_6_not_q, nor_1_out, not_1_out, not_2_out;

  not not_1 (not_1_out, CLK);
  D_latch d_latch_1 (.EN(CLK), .D(_3_out), .Q(d_latch_1_q));  // open: NOT_Q
  D_latch d_latch_2 (.EN(not_1_out), .D(nor_1_out), .NOT_Q(d_latch_2_not_q));  // open: Q
  nor nor_1 (nor_1_out, d_latch_1_q, RES);
  D_latch d_latch_3 (.EN(CLK), .D(d_latch_2_not_q), .NOT_Q(d_latch_3_not_q));  // open: Q
  D_latch d_latch_4 (.EN(not_1_out), .D(d_latch_3_not_q), .NOT_Q(d_latch_4_not_q));  // open: Q
  D_latch d_latch_5 (.EN(CLK), .D(d_latch_4_not_q), .NOT_Q(d_latch_5_not_q));  // open: Q
  D_latch d_latch_6 (.EN(not_1_out), .D(d_latch_5_not_q), .NOT_Q(d_latch_6_not_q));  // open: Q
  not not_2 (not_2_out, d_latch_5_not_q);
  nor _2 (_2_out, d_latch_6_not_q, not_2_out);
  nor _3 (_3_out, d_latch_6_not_q, d_latch_4_not_q);
  not not_3 (PCLK, _2_out);

  // Notes on the sheet:
  //   9
  //   8
  //   Pixel clock is disabled during RESET (PPU stall)
  //   7
  //   6
  //   5
  //   4
  //   1
  //   PCLK = CLK / 5
  //   !
endmodule

module RESET_FF (
  input  nRES,
  input  RESCL,
  output RES,
  output RC
);

  wire nor_1_out;

  not not_1 (RES, nRES);
  nor nor_1 (nor_1_out, RES, RC);
  nor nor_2 (RC, nor_1_out, RESCL);

  // Notes on the sheet:
  //   Reset flip/flop remains set after RESET, until not cleared by RESCL
  //   Reset flip/flop
  //   (REG CLEAR)
endmodule

module COUNTER_BIT (
  input  CLK,
  input  in,
  input  RES,
  input  clear,
  output OUT,
  output PROP_DELAY_OUT,
  output carry_out
);

  wire d_latch_1_q, multiplexer_1_out, multiplexer_2_out, nor_3_out, not_2_out, not_3_out;

  not not_1 (PROP_DELAY_OUT, multiplexer_1_out);
  nor nor_1 (OUT, PROP_DELAY_OUT, RES);
  nor nor_2 (carry_out, PROP_DELAY_OUT, not_2_out);
  not not_2 (not_2_out, in);
  Multiplexer #(.enable("false")) multiplexer_1 (.in0(OUT), .in1(nor_3_out), .out(multiplexer_1_out), .sel(CLK));
  not not_3 (not_3_out, CLK);
  Multiplexer #(.enable("false")) multiplexer_2 (.in0(PROP_DELAY_OUT), .in1(OUT), .out(multiplexer_2_out), .sel(in));
  nor nor_3 (nor_3_out, d_latch_1_q, clear);
  D_latch d_latch_1 (.EN(not_3_out), .D(multiplexer_2_out), .Q(d_latch_1_q));  // open: NOT_Q

  // Notes on the sheet:
  //   carry_in
  //   global RESET
  //   clear manually
endmodule

module H_COUNTER (
  input  RES,
  input  HC,
  input  CLK,
  output H0,
  output H1,
  output H2,
  output H3,
  output H4,
  output H5,
  output H6,
  output H7,
  output H8
);

  wire counter_bit_1_carry_out, counter_bit_1_prop_delay_out, counter_bit_2_carry_out,
       counter_bit_2_prop_delay_out, counter_bit_3_carry_out, counter_bit_3_prop_delay_out,
       counter_bit_4_carry_out, counter_bit_4_prop_delay_out, counter_bit_5_prop_delay_out,
       counter_bit_6_carry_out, counter_bit_6_prop_delay_out, counter_bit_7_carry_out,
       counter_bit_7_prop_delay_out, counter_bit_8_carry_out, counter_bit_8_prop_delay_out,
       counter_bit_9_prop_delay_out, nor_1_out;

  COUNTER_BIT counter_bit_1 (
    .in(1'b1), .CLK(CLK), .clear(HC), .RES(RES), .OUT(H0), .carry_out(counter_bit_1_carry_out),
    .PROP_DELAY_OUT(counter_bit_1_prop_delay_out));
  COUNTER_BIT counter_bit_2 (
    .in(counter_bit_1_carry_out), .CLK(CLK), .clear(HC), .RES(RES), .OUT(H1),
    .carry_out(counter_bit_2_carry_out), .PROP_DELAY_OUT(counter_bit_2_prop_delay_out));
  COUNTER_BIT counter_bit_3 (
    .in(counter_bit_2_carry_out), .CLK(CLK), .clear(HC), .RES(RES), .OUT(H2),
    .carry_out(counter_bit_3_carry_out), .PROP_DELAY_OUT(counter_bit_3_prop_delay_out));
  COUNTER_BIT counter_bit_4 (
    .in(counter_bit_3_carry_out), .CLK(CLK), .clear(HC), .RES(RES), .OUT(H3),
    .carry_out(counter_bit_4_carry_out), .PROP_DELAY_OUT(counter_bit_4_prop_delay_out));
  COUNTER_BIT counter_bit_5 (
    .in(counter_bit_4_carry_out), .CLK(CLK), .clear(HC), .RES(RES), .OUT(H4),
    .PROP_DELAY_OUT(counter_bit_5_prop_delay_out));  // open: carry_out
  COUNTER_BIT counter_bit_6 (
    .in(nor_1_out), .CLK(CLK), .clear(HC), .RES(RES), .OUT(H5), .carry_out(counter_bit_6_carry_out),
    .PROP_DELAY_OUT(counter_bit_6_prop_delay_out));
  COUNTER_BIT counter_bit_7 (
    .in(counter_bit_6_carry_out), .CLK(CLK), .clear(HC), .RES(RES), .OUT(H6),
    .carry_out(counter_bit_7_carry_out), .PROP_DELAY_OUT(counter_bit_7_prop_delay_out));
  COUNTER_BIT counter_bit_8 (
    .in(counter_bit_7_carry_out), .CLK(CLK), .clear(HC), .RES(RES), .OUT(H7),
    .carry_out(counter_bit_8_carry_out), .PROP_DELAY_OUT(counter_bit_8_prop_delay_out));
  COUNTER_BIT counter_bit_9 (
    .in(counter_bit_8_carry_out), .CLK(CLK), .clear(HC), .RES(RES), .OUT(H8),
    .PROP_DELAY_OUT(counter_bit_9_prop_delay_out));  // open: carry_out
  nor nor_1 (nor_1_out, counter_bit_5_prop_delay_out, counter_bit_4_prop_delay_out, counter_bit_3_prop_delay_out, counter_bit_2_prop_delay_out, counter_bit_1_prop_delay_out);

  // Notes on the sheet:
  //   reduce propagation delay
endmodule

module V_COUNTER (
  input  VIN,
  input  CLK,
  input  RES,
  input  VC,
  output V0,
  output V1,
  output V2,
  output V3,
  output V4,
  output V5,
  output V6,
  output V7,
  output V8
);

  wire counter_bit_1_carry_out, counter_bit_1_prop_delay_out, counter_bit_2_carry_out,
       counter_bit_2_prop_delay_out, counter_bit_3_carry_out, counter_bit_3_prop_delay_out,
       counter_bit_4_carry_out, counter_bit_4_prop_delay_out, counter_bit_5_prop_delay_out,
       counter_bit_6_carry_out, counter_bit_6_prop_delay_out, counter_bit_7_carry_out,
       counter_bit_7_prop_delay_out, counter_bit_8_carry_out, counter_bit_8_prop_delay_out,
       counter_bit_9_prop_delay_out, nor_1_out, not_1_out;

  COUNTER_BIT counter_bit_1 (
    .in(VIN), .CLK(CLK), .clear(RES), .RES(VC), .OUT(V0), .carry_out(counter_bit_1_carry_out),
    .PROP_DELAY_OUT(counter_bit_1_prop_delay_out));
  COUNTER_BIT counter_bit_2 (
    .in(counter_bit_1_carry_out), .CLK(CLK), .clear(RES), .RES(VC), .OUT(V1),
    .carry_out(counter_bit_2_carry_out), .PROP_DELAY_OUT(counter_bit_2_prop_delay_out));
  COUNTER_BIT counter_bit_3 (
    .in(counter_bit_2_carry_out), .CLK(CLK), .clear(RES), .RES(VC), .OUT(V2),
    .carry_out(counter_bit_3_carry_out), .PROP_DELAY_OUT(counter_bit_3_prop_delay_out));
  COUNTER_BIT counter_bit_4 (
    .in(counter_bit_3_carry_out), .CLK(CLK), .clear(RES), .RES(VC), .OUT(V3),
    .carry_out(counter_bit_4_carry_out), .PROP_DELAY_OUT(counter_bit_4_prop_delay_out));
  COUNTER_BIT counter_bit_5 (
    .in(counter_bit_4_carry_out), .CLK(CLK), .clear(RES), .RES(VC), .OUT(V4),
    .PROP_DELAY_OUT(counter_bit_5_prop_delay_out));  // open: carry_out
  COUNTER_BIT counter_bit_6 (
    .in(nor_1_out), .CLK(CLK), .clear(RES), .RES(VC), .OUT(V5), .carry_out(counter_bit_6_carry_out),
    .PROP_DELAY_OUT(counter_bit_6_prop_delay_out));
  COUNTER_BIT counter_bit_7 (
    .in(counter_bit_6_carry_out), .CLK(CLK), .clear(RES), .RES(VC), .OUT(V6),
    .carry_out(counter_bit_7_carry_out), .PROP_DELAY_OUT(counter_bit_7_prop_delay_out));
  COUNTER_BIT counter_bit_8 (
    .in(counter_bit_7_carry_out), .CLK(CLK), .clear(RES), .RES(VC), .OUT(V7),
    .carry_out(counter_bit_8_carry_out), .PROP_DELAY_OUT(counter_bit_8_prop_delay_out));
  COUNTER_BIT counter_bit_9 (
    .in(counter_bit_8_carry_out), .CLK(CLK), .clear(RES), .RES(VC), .OUT(V8),
    .PROP_DELAY_OUT(counter_bit_9_prop_delay_out));  // open: carry_out
  not not_1 (not_1_out, VIN);
  nor nor_1 (nor_1_out, counter_bit_5_prop_delay_out, counter_bit_4_prop_delay_out, counter_bit_3_prop_delay_out, counter_bit_2_prop_delay_out, counter_bit_1_prop_delay_out, not_1_out);

  // Notes on the sheet:
  //   reduce propagation delay
endmodule

module HV_SELECT (
  input  H8,
  input  H7,
  input  H6,
  input  H5,
  input  H4,
  input  H3,
  input  H2,
  input  H1,
  input  H0,
  input  VB,
  input  BLNK,
  input  V8,
  input  V7,
  input  V6,
  input  V5,
  input  V4,
  input  V3,
  input  V2,
  input  V1,
  input  V0,
  output [5:0] Hnn,
  output _277,
  output _256,
  output _65,
  output _0_7__256_263,
  output _0_255,
  output _339,
  output _63,
  output _255,
  output _0_63,
  output _256_319,
  output _0_255_2,
  output _0_1,
  output _6_7,
  output _4_5,
  output _320_355,
  output _0___255,
  output _2_3,
  output _256_2,
  output _4,
  output _277_2,
  output _302,
  output _321,
  output _306,
  output _340,
  output [7:0] VPOS,
  output _272,
  output _269,
  output _1,
  output _240,
  output _241,
  output _0,
  output _240_2,
  output _311,
  output _311_2,
  output _265
);

  wire not_1_out, not_2_out, not_3_out, not_4_out, not_5_out, not_6_out, not_7_out, not_8_out, not_9_out,
       not_10_out, not_11_out, not_12_out, not_13_out, not_14_out, not_15_out, not_16_out, not_17_out,
       not_18_out;

  not not_1 (not_1_out, H8);
  not not_2 (not_2_out, H7);
  not not_3 (not_3_out, H6);
  not not_4 (not_4_out, H5);
  not not_5 (not_5_out, H4);
  not not_6 (not_6_out, H3);
  not not_7 (not_7_out, H2);
  not not_8 (not_8_out, H1);
  not not_9 (not_9_out, H0);
  not not_10 (not_10_out, V8);
  not not_11 (not_11_out, V7);
  not not_12 (not_12_out, V6);
  not not_13 (not_13_out, V5);
  not not_14 (not_14_out, V4);
  not not_15 (not_15_out, V3);
  not not_16 (not_16_out, V2);
  not not_17 (not_17_out, V1);
  not not_18 (not_18_out, V0);
  Pull_Resistor #(.pull(1)) pull_resistor_1 (.node(_277));
  Transistor #(.\type ("n")) transistor_1 (.in(1'b0), .out(_277), .gate(not_1_out));
  Transistor #(.\type ("n")) transistor_2 (.in(1'b0), .out(_277), .gate(H7));
  Transistor #(.\type ("n")) transistor_3 (.in(1'b0), .out(_277), .gate(H6));
  Transistor #(.\type ("n")) transistor_4 (.in(1'b0), .out(_277), .gate(H5));
  Transistor #(.\type ("n")) transistor_5 (.in(1'b0), .out(_277), .gate(not_5_out));
  Transistor #(.\type ("n")) transistor_6 (.in(1'b0), .out(_277), .gate(H3));
  Transistor #(.\type ("n")) transistor_7 (.in(1'b0), .out(_277), .gate(not_7_out));
  Transistor #(.\type ("n")) transistor_8 (.in(1'b0), .out(_277), .gate(H1));
  Transistor #(.\type ("n")) transistor_9 (.in(1'b0), .out(_277), .gate(not_9_out));
  Pull_Resistor #(.pull(1)) pull_resistor_2 (.node(_272));
  Transistor #(.\type ("n")) transistor_10 (.in(1'b0), .out(_272), .gate(not_10_out));
  Transistor #(.\type ("n")) transistor_11 (.in(1'b0), .out(_272), .gate(V7));
  Transistor #(.\type ("n")) transistor_12 (.in(1'b0), .out(_272), .gate(V6));
  Transistor #(.\type ("n")) transistor_13 (.in(1'b0), .out(_272), .gate(V5));
  Transistor #(.\type ("n")) transistor_14 (.in(1'b0), .out(_272), .gate(not_14_out));
  Transistor #(.\type ("n")) transistor_15 (.in(1'b0), .out(_272), .gate(V3));
  Transistor #(.\type ("n")) transistor_16 (.in(1'b0), .out(_272), .gate(V2));
  Transistor #(.\type ("n")) transistor_17 (.in(1'b0), .out(_272), .gate(V1));
  Transistor #(.\type ("n")) transistor_18 (.in(1'b0), .out(_272), .gate(V0));
  Pull_Resistor #(.pull(1)) pull_resistor_3 (.node(_256));
  Transistor #(.\type ("n")) transistor_19 (.in(1'b0), .out(_256), .gate(not_1_out));
  Transistor #(.\type ("n")) transistor_20 (.in(1'b0), .out(_256), .gate(H7));
  Transistor #(.\type ("n")) transistor_21 (.in(1'b0), .out(_256), .gate(H6));
  Transistor #(.\type ("n")) transistor_22 (.in(1'b0), .out(_256), .gate(H5));
  Transistor #(.\type ("n")) transistor_23 (.in(1'b0), .out(_256), .gate(H4));
  Transistor #(.\type ("n")) transistor_24 (.in(1'b0), .out(_256), .gate(H3));
  Transistor #(.\type ("n")) transistor_25 (.in(1'b0), .out(_256), .gate(H2));
  Transistor #(.\type ("n")) transistor_26 (.in(1'b0), .out(_256), .gate(H1));
  Transistor #(.\type ("n")) transistor_27 (.in(1'b0), .out(_256), .gate(H0));
  Pull_Resistor #(.pull(1)) pull_resistor_4 (.node(_269));
  Transistor #(.\type ("n")) transistor_28 (.in(1'b0), .out(_269), .gate(not_10_out));
  Transistor #(.\type ("n")) transistor_29 (.in(1'b0), .out(_269), .gate(V7));
  Transistor #(.\type ("n")) transistor_30 (.in(1'b0), .out(_269), .gate(V6));
  Transistor #(.\type ("n")) transistor_31 (.in(1'b0), .out(_269), .gate(V5));
  Transistor #(.\type ("n")) transistor_32 (.in(1'b0), .out(_269), .gate(V4));
  Transistor #(.\type ("n")) transistor_33 (.in(1'b0), .out(_269), .gate(not_15_out));
  Transistor #(.\type ("n")) transistor_34 (.in(1'b0), .out(_269), .gate(not_16_out));
  Transistor #(.\type ("n")) transistor_35 (.in(1'b0), .out(_269), .gate(V1));
  Transistor #(.\type ("n")) transistor_36 (.in(1'b0), .out(_269), .gate(not_18_out));
  Pull_Resistor #(.pull(1)) pull_resistor_5 (.node(_65));
  Transistor #(.\type ("n")) transistor_37 (.in(1'b0), .out(_65), .gate(H8));
  Transistor #(.\type ("n")) transistor_38 (.in(1'b0), .out(_65), .gate(H7));
  Transistor #(.\type ("n")) transistor_39 (.in(1'b0), .out(_65), .gate(not_3_out));
  Transistor #(.\type ("n")) transistor_40 (.in(1'b0), .out(_65), .gate(H5));
  Transistor #(.\type ("n")) transistor_41 (.in(1'b0), .out(_65), .gate(H4));
  Transistor #(.\type ("n")) transistor_42 (.in(1'b0), .out(_65), .gate(H3));
  Transistor #(.\type ("n")) transistor_43 (.in(1'b0), .out(_65), .gate(H2));
  Transistor #(.\type ("n")) transistor_44 (.in(1'b0), .out(_65), .gate(H1));
  Transistor #(.\type ("n")) transistor_45 (.in(1'b0), .out(_65), .gate(not_9_out));
  Transistor #(.\type ("n")) transistor_46 (.in(1'b0), .out(_65), .gate(BLNK));
  Pull_Resistor #(.pull(1)) pull_resistor_6 (.node(_1));
  Transistor #(.\type ("n")) transistor_47 (.in(1'b0), .out(_1), .gate(V8));
  Transistor #(.\type ("n")) transistor_48 (.in(1'b0), .out(_1), .gate(V7));
  Transistor #(.\type ("n")) transistor_49 (.in(1'b0), .out(_1), .gate(V6));
  Transistor #(.\type ("n")) transistor_50 (.in(1'b0), .out(_1), .gate(V5));
  Transistor #(.\type ("n")) transistor_51 (.in(1'b0), .out(_1), .gate(V4));
  Transistor #(.\type ("n")) transistor_52 (.in(1'b0), .out(_1), .gate(V3));
  Transistor #(.\type ("n")) transistor_53 (.in(1'b0), .out(_1), .gate(V2));
  Transistor #(.\type ("n")) transistor_54 (.in(1'b0), .out(_1), .gate(V1));
  Transistor #(.\type ("n")) transistor_55 (.in(1'b0), .out(_1), .gate(not_18_out));
  Pull_Resistor #(.pull(1)) pull_resistor_7 (.node(_0_7__256_263));
  Transistor #(.\type ("n")) transistor_56 (.in(1'b0), .out(_0_7__256_263), .gate(H7));
  Transistor #(.\type ("n")) transistor_57 (.in(1'b0), .out(_0_7__256_263), .gate(H6));
  Transistor #(.\type ("n")) transistor_58 (.in(1'b0), .out(_0_7__256_263), .gate(H5));
  Transistor #(.\type ("n")) transistor_59 (.in(1'b0), .out(_0_7__256_263), .gate(H4));
  Transistor #(.\type ("n")) transistor_60 (.in(1'b0), .out(_0_7__256_263), .gate(H3));
  Pull_Resistor #(.pull(1)) pull_resistor_8 (.node(_240));
  Transistor #(.\type ("n")) transistor_61 (.in(1'b0), .out(_240), .gate(not_11_out));
  Transistor #(.\type ("n")) transistor_62 (.in(1'b0), .out(_240), .gate(not_12_out));
  Transistor #(.\type ("n")) transistor_63 (.in(1'b0), .out(_240), .gate(not_13_out));
  Transistor #(.\type ("n")) transistor_64 (.in(1'b0), .out(_240), .gate(not_14_out));
  Transistor #(.\type ("n")) transistor_65 (.in(1'b0), .out(_240), .gate(V3));
  Transistor #(.\type ("n")) transistor_66 (.in(1'b0), .out(_240), .gate(V2));
  Transistor #(.\type ("n")) transistor_67 (.in(1'b0), .out(_240), .gate(V1));
  Transistor #(.\type ("n")) transistor_68 (.in(1'b0), .out(_240), .gate(V0));
  Pull_Resistor #(.pull(1)) pull_resistor_9 (.node(_339));
  Pull_Resistor #(.pull(1)) pull_resistor_10 (.node(_0_255));
  Transistor #(.\type ("n")) transistor_69 (.in(1'b0), .out(_0_255), .gate(H8));
  Transistor #(.\type ("n")) transistor_70 (.in(1'b0), .out(_339), .gate(not_1_out));
  Transistor #(.\type ("n")) transistor_71 (.in(1'b0), .out(_339), .gate(H7));
  Transistor #(.\type ("n")) transistor_72 (.in(1'b0), .out(_339), .gate(not_3_out));
  Transistor #(.\type ("n")) transistor_73 (.in(1'b0), .out(_339), .gate(H5));
  Transistor #(.\type ("n")) transistor_74 (.in(1'b0), .out(_339), .gate(not_5_out));
  Transistor #(.\type ("n")) transistor_75 (.in(1'b0), .out(_339), .gate(H3));
  Transistor #(.\type ("n")) transistor_76 (.in(1'b0), .out(_339), .gate(H2));
  Transistor #(.\type ("n")) transistor_77 (.in(1'b0), .out(_339), .gate(not_8_out));
  Transistor #(.\type ("n")) transistor_78 (.in(1'b0), .out(_339), .gate(not_9_out));
  Transistor #(.\type ("n")) transistor_79 (.in(1'b0), .out(_0_255), .gate(VB));
  Transistor #(.\type ("n")) transistor_80 (.in(1'b0), .out(_339), .gate(BLNK));
  Pull_Resistor #(.pull(1)) pull_resistor_11 (.node(_241));
  Pull_Resistor #(.pull(1)) pull_resistor_12 (.node(_0));
  Transistor #(.\type ("n")) transistor_81 (.in(1'b0), .out(_0), .gate(V8));
  Transistor #(.\type ("n")) transistor_82 (.in(1'b0), .out(_0), .gate(V7));
  Transistor #(.\type ("n")) transistor_83 (.in(1'b0), .out(_241), .gate(not_11_out));
  Transistor #(.\type ("n")) transistor_84 (.in(1'b0), .out(_0), .gate(V6));
  Transistor #(.\type ("n")) transistor_85 (.in(1'b0), .out(_241), .gate(not_12_out));
  Transistor #(.\type ("n")) transistor_86 (.in(1'b0), .out(_0), .gate(V5));
  Transistor #(.\type ("n")) transistor_87 (.in(1'b0), .out(_241), .gate(not_13_out));
  Transistor #(.\type ("n")) transistor_88 (.in(1'b0), .out(_0), .gate(V4));
  Transistor #(.\type ("n")) transistor_89 (.in(1'b0), .out(_241), .gate(not_14_out));
  Transistor #(.\type ("n")) transistor_90 (.in(1'b0), .out(_241), .gate(V3));
  Transistor #(.\type ("n")) transistor_91 (.in(1'b0), .out(_0), .gate(V3));
  Transistor #(.\type ("n")) transistor_92 (.in(1'b0), .out(_241), .gate(V2));
  Transistor #(.\type ("n")) transistor_93 (.in(1'b0), .out(_0), .gate(V2));
  Transistor #(.\type ("n")) transistor_94 (.in(1'b0), .out(_0), .gate(V1));
  Transistor #(.\type ("n")) transistor_95 (.in(1'b0), .out(_241), .gate(V1));
  Transistor #(.\type ("n")) transistor_96 (.in(1'b0), .out(_0), .gate(V0));
  Transistor #(.\type ("n")) transistor_97 (.in(1'b0), .out(_241), .gate(not_18_out));
  Pull_Resistor #(.pull(1)) pull_resistor_13 (.node(_63));
  Transistor #(.\type ("n")) transistor_98 (.in(1'b0), .out(_63), .gate(H8));
  Transistor #(.\type ("n")) transistor_99 (.in(1'b0), .out(_63), .gate(H7));
  Transistor #(.\type ("n")) transistor_100 (.in(1'b0), .out(_63), .gate(H6));
  Transistor #(.\type ("n")) transistor_101 (.in(1'b0), .out(_63), .gate(not_4_out));
  Transistor #(.\type ("n")) transistor_102 (.in(1'b0), .out(_63), .gate(not_5_out));
  Transistor #(.\type ("n")) transistor_103 (.in(1'b0), .out(_63), .gate(not_6_out));
  Transistor #(.\type ("n")) transistor_104 (.in(1'b0), .out(_63), .gate(not_7_out));
  Transistor #(.\type ("n")) transistor_105 (.in(1'b0), .out(_63), .gate(not_8_out));
  Transistor #(.\type ("n")) transistor_106 (.in(1'b0), .out(_63), .gate(not_9_out));
  Transistor #(.\type ("n")) transistor_107 (.in(1'b0), .out(_63), .gate(BLNK));
  Pull_Resistor #(.pull(1)) pull_resistor_14 (.node(_240_2));
  Transistor #(.\type ("n")) transistor_108 (.in(1'b0), .out(_240_2), .gate(not_11_out));
  Transistor #(.\type ("n")) transistor_109 (.in(1'b0), .out(_240_2), .gate(not_12_out));
  Transistor #(.\type ("n")) transistor_110 (.in(1'b0), .out(_240_2), .gate(not_13_out));
  Transistor #(.\type ("n")) transistor_111 (.in(1'b0), .out(_240_2), .gate(not_14_out));
  Transistor #(.\type ("n")) transistor_112 (.in(1'b0), .out(_240_2), .gate(V3));
  Transistor #(.\type ("n")) transistor_113 (.in(1'b0), .out(_240_2), .gate(V2));
  Transistor #(.\type ("n")) transistor_114 (.in(1'b0), .out(_240_2), .gate(V1));
  Transistor #(.\type ("n")) transistor_115 (.in(1'b0), .out(_240_2), .gate(V0));
  Pull_Resistor #(.pull(1)) pull_resistor_15 (.node(_255));
  Transistor #(.\type ("n")) transistor_116 (.in(1'b0), .out(_255), .gate(not_2_out));
  Transistor #(.\type ("n")) transistor_117 (.in(1'b0), .out(_255), .gate(not_3_out));
  Transistor #(.\type ("n")) transistor_118 (.in(1'b0), .out(_255), .gate(not_4_out));
  Transistor #(.\type ("n")) transistor_119 (.in(1'b0), .out(_255), .gate(not_5_out));
  Transistor #(.\type ("n")) transistor_120 (.in(1'b0), .out(_255), .gate(not_6_out));
  Transistor #(.\type ("n")) transistor_121 (.in(1'b0), .out(_255), .gate(not_7_out));
  Transistor #(.\type ("n")) transistor_122 (.in(1'b0), .out(_255), .gate(not_8_out));
  Transistor #(.\type ("n")) transistor_123 (.in(1'b0), .out(_255), .gate(not_9_out));
  Transistor #(.\type ("n")) transistor_124 (.in(1'b0), .out(_255), .gate(BLNK));
  Pull_Resistor #(.pull(1)) pull_resistor_16 (.node(_311));
  Transistor #(.\type ("n")) transistor_125 (.in(1'b0), .out(_311), .gate(not_10_out));
  Transistor #(.\type ("n")) transistor_126 (.in(1'b0), .out(_311), .gate(V7));
  Transistor #(.\type ("n")) transistor_127 (.in(1'b0), .out(_311), .gate(V6));
  Transistor #(.\type ("n")) transistor_128 (.in(1'b0), .out(_311), .gate(not_13_out));
  Transistor #(.\type ("n")) transistor_129 (.in(1'b0), .out(_311), .gate(not_14_out));
  Transistor #(.\type ("n")) transistor_130 (.in(1'b0), .out(_311), .gate(V3));
  Transistor #(.\type ("n")) transistor_131 (.in(1'b0), .out(_311), .gate(not_16_out));
  Transistor #(.\type ("n")) transistor_132 (.in(1'b0), .out(_311), .gate(not_17_out));
  Transistor #(.\type ("n")) transistor_133 (.in(1'b0), .out(_311), .gate(not_18_out));
  Pull_Resistor #(.pull(1)) pull_resistor_17 (.node(_0_63));
  Transistor #(.\type ("n")) transistor_134 (.in(1'b0), .out(_0_63), .gate(H8));
  Transistor #(.\type ("n")) transistor_135 (.in(1'b0), .out(_0_63), .gate(H7));
  Transistor #(.\type ("n")) transistor_136 (.in(1'b0), .out(_0_63), .gate(H6));
  Transistor #(.\type ("n")) transistor_137 (.in(1'b0), .out(_0_63), .gate(BLNK));
  Pull_Resistor #(.pull(1)) pull_resistor_18 (.node(_311_2));
  Transistor #(.\type ("n")) transistor_138 (.in(1'b0), .out(_311_2), .gate(not_10_out));
  Transistor #(.\type ("n")) transistor_139 (.in(1'b0), .out(_311_2), .gate(V7));
  Transistor #(.\type ("n")) transistor_140 (.in(1'b0), .out(_311_2), .gate(V6));
  Transistor #(.\type ("n")) transistor_141 (.in(1'b0), .out(_311_2), .gate(not_13_out));
  Transistor #(.\type ("n")) transistor_142 (.in(1'b0), .out(_311_2), .gate(not_14_out));
  Transistor #(.\type ("n")) transistor_143 (.in(1'b0), .out(_311_2), .gate(V3));
  Transistor #(.\type ("n")) transistor_144 (.in(1'b0), .out(_311_2), .gate(not_16_out));
  Transistor #(.\type ("n")) transistor_145 (.in(1'b0), .out(_311_2), .gate(not_17_out));
  Transistor #(.\type ("n")) transistor_146 (.in(1'b0), .out(_311_2), .gate(not_18_out));
  Pull_Resistor #(.pull(1)) pull_resistor_19 (.node(_256_319));
  Transistor #(.\type ("n")) transistor_147 (.in(1'b0), .out(_256_319), .gate(not_1_out));
  Transistor #(.\type ("n")) transistor_148 (.in(1'b0), .out(_256_319), .gate(H7));
  Transistor #(.\type ("n")) transistor_149 (.in(1'b0), .out(_256_319), .gate(H6));
  Transistor #(.\type ("n")) transistor_150 (.in(1'b0), .out(_256_319), .gate(BLNK));
  Pull_Resistor #(.pull(1)) pull_resistor_20 (.node(_265));
  Transistor #(.\type ("n")) transistor_151 (.in(1'b0), .out(_265), .gate(not_10_out));
  Transistor #(.\type ("n")) transistor_152 (.in(1'b0), .out(_265), .gate(V7));
  Transistor #(.\type ("n")) transistor_153 (.in(1'b0), .out(_265), .gate(V6));
  Transistor #(.\type ("n")) transistor_154 (.in(1'b0), .out(_265), .gate(V5));
  Transistor #(.\type ("n")) transistor_155 (.in(1'b0), .out(_265), .gate(V4));
  Transistor #(.\type ("n")) transistor_156 (.in(1'b0), .out(_265), .gate(not_15_out));
  Transistor #(.\type ("n")) transistor_157 (.in(1'b0), .out(_265), .gate(V2));
  Transistor #(.\type ("n")) transistor_158 (.in(1'b0), .out(_265), .gate(V1));
  Transistor #(.\type ("n")) transistor_159 (.in(1'b0), .out(_265), .gate(not_18_out));
  Pull_Resistor #(.pull(1)) pull_resistor_21 (.node(_0_255_2));
  Transistor #(.\type ("n")) transistor_160 (.in(1'b0), .out(_0_255_2), .gate(H8));
  Transistor #(.\type ("n")) transistor_161 (.in(1'b0), .out(_0_255_2), .gate(VB));
  Transistor #(.\type ("n")) transistor_162 (.in(1'b0), .out(_0_255_2), .gate(BLNK));
  Pull_Resistor #(.pull(1)) pull_resistor_22 (.node(_0_1));
  Transistor #(.\type ("n")) transistor_163 (.in(1'b0), .out(_0_1), .gate(H2));
  Transistor #(.\type ("n")) transistor_164 (.in(1'b0), .out(_0_1), .gate(H1));
  Transistor #(.\type ("n")) transistor_165 (.in(1'b0), .out(_0_1), .gate(BLNK));
  Pull_Resistor #(.pull(1)) pull_resistor_23 (.node(_4_5));
  Pull_Resistor #(.pull(1)) pull_resistor_24 (.node(_6_7));
  Transistor #(.\type ("n")) transistor_166 (.in(1'b0), .out(_6_7), .gate(not_7_out));
  Transistor #(.\type ("n")) transistor_167 (.in(1'b0), .out(_4_5), .gate(not_7_out));
  Transistor #(.\type ("n")) transistor_168 (.in(1'b0), .out(_4_5), .gate(H1));
  Transistor #(.\type ("n")) transistor_169 (.in(1'b0), .out(_6_7), .gate(not_8_out));
  Pull_Resistor #(.pull(1)) pull_resistor_25 (.node(_320_355));
  Transistor #(.\type ("n")) transistor_170 (.in(1'b0), .out(_320_355), .gate(not_1_out));
  Transistor #(.\type ("n")) transistor_171 (.in(1'b0), .out(_320_355), .gate(not_3_out));
  Transistor #(.\type ("n")) transistor_172 (.in(1'b0), .out(_320_355), .gate(H5));
  Transistor #(.\type ("n")) transistor_173 (.in(1'b0), .out(_320_355), .gate(H4));
  Transistor #(.\type ("n")) transistor_174 (.in(1'b0), .out(_320_355), .gate(BLNK));
  Pull_Resistor #(.pull(1)) pull_resistor_26 (.node(_0___255));
  Transistor #(.\type ("n")) transistor_175 (.in(1'b0), .out(_0___255), .gate(H8));
  Transistor #(.\type ("n")) transistor_176 (.in(1'b0), .out(_0___255), .gate(BLNK));
  Pull_Resistor #(.pull(1)) pull_resistor_27 (.node(_2_3));
  Transistor #(.\type ("n")) transistor_177 (.in(1'b0), .out(_2_3), .gate(H2));
  Transistor #(.\type ("n")) transistor_178 (.in(1'b0), .out(_2_3), .gate(not_8_out));
  Pull_Resistor #(.pull(1)) pull_resistor_28 (.node(_256_2));
  Transistor #(.\type ("n")) transistor_179 (.in(1'b0), .out(_256_2), .gate(not_1_out));
  Transistor #(.\type ("n")) transistor_180 (.in(1'b0), .out(_256_2), .gate(H7));
  Transistor #(.\type ("n")) transistor_181 (.in(1'b0), .out(_256_2), .gate(H6));
  Transistor #(.\type ("n")) transistor_182 (.in(1'b0), .out(_256_2), .gate(H5));
  Transistor #(.\type ("n")) transistor_183 (.in(1'b0), .out(_256_2), .gate(H4));
  Transistor #(.\type ("n")) transistor_184 (.in(1'b0), .out(_256_2), .gate(H3));
  Transistor #(.\type ("n")) transistor_185 (.in(1'b0), .out(_256_2), .gate(H2));
  Transistor #(.\type ("n")) transistor_186 (.in(1'b0), .out(_256_2), .gate(H1));
  Transistor #(.\type ("n")) transistor_187 (.in(1'b0), .out(_256_2), .gate(H0));
  Pull_Resistor #(.pull(1)) pull_resistor_29 (.node(_4));
  Transistor #(.\type ("n")) transistor_188 (.in(1'b0), .out(_4), .gate(H8));
  Transistor #(.\type ("n")) transistor_189 (.in(1'b0), .out(_4), .gate(H7));
  Transistor #(.\type ("n")) transistor_190 (.in(1'b0), .out(_4), .gate(H6));
  Transistor #(.\type ("n")) transistor_191 (.in(1'b0), .out(_4), .gate(H5));
  Transistor #(.\type ("n")) transistor_192 (.in(1'b0), .out(_4), .gate(H4));
  Transistor #(.\type ("n")) transistor_193 (.in(1'b0), .out(_4), .gate(H3));
  Transistor #(.\type ("n")) transistor_194 (.in(1'b0), .out(_4), .gate(not_7_out));
  Transistor #(.\type ("n")) transistor_195 (.in(1'b0), .out(_4), .gate(H1));
  Transistor #(.\type ("n")) transistor_196 (.in(1'b0), .out(_4), .gate(H0));
  Pull_Resistor #(.pull(1)) pull_resistor_30 (.node(_277_2));
  Transistor #(.\type ("n")) transistor_197 (.in(1'b0), .out(_277_2), .gate(not_1_out));
  Transistor #(.\type ("n")) transistor_198 (.in(1'b0), .out(_277_2), .gate(H7));
  Transistor #(.\type ("n")) transistor_199 (.in(1'b0), .out(_277_2), .gate(H6));
  Transistor #(.\type ("n")) transistor_200 (.in(1'b0), .out(_277_2), .gate(H5));
  Transistor #(.\type ("n")) transistor_201 (.in(1'b0), .out(_277_2), .gate(not_5_out));
  Transistor #(.\type ("n")) transistor_202 (.in(1'b0), .out(_277_2), .gate(H3));
  Transistor #(.\type ("n")) transistor_203 (.in(1'b0), .out(_277_2), .gate(not_7_out));
  Transistor #(.\type ("n")) transistor_204 (.in(1'b0), .out(_277_2), .gate(H1));
  Transistor #(.\type ("n")) transistor_205 (.in(1'b0), .out(_277_2), .gate(not_9_out));
  Pull_Resistor #(.pull(1)) pull_resistor_31 (.node(_321));
  Pull_Resistor #(.pull(1)) pull_resistor_32 (.node(_302));
  Transistor #(.\type ("n")) transistor_206 (.in(1'b0), .out(_321), .gate(not_1_out));
  Transistor #(.\type ("n")) transistor_207 (.in(1'b0), .out(_302), .gate(not_1_out));
  Transistor #(.\type ("n")) transistor_208 (.in(1'b0), .out(_302), .gate(H7));
  Transistor #(.\type ("n")) transistor_209 (.in(1'b0), .out(_321), .gate(H7));
  Transistor #(.\type ("n")) transistor_210 (.in(1'b0), .out(_302), .gate(H6));
  Transistor #(.\type ("n")) transistor_211 (.in(1'b0), .out(_321), .gate(not_3_out));
  Transistor #(.\type ("n")) transistor_212 (.in(1'b0), .out(_321), .gate(H5));
  Transistor #(.\type ("n")) transistor_213 (.in(1'b0), .out(_302), .gate(not_4_out));
  Transistor #(.\type ("n")) transistor_214 (.in(1'b0), .out(_302), .gate(H4));
  Transistor #(.\type ("n")) transistor_215 (.in(1'b0), .out(_321), .gate(H4));
  Transistor #(.\type ("n")) transistor_216 (.in(1'b0), .out(_321), .gate(H3));
  Transistor #(.\type ("n")) transistor_217 (.in(1'b0), .out(_302), .gate(not_6_out));
  Transistor #(.\type ("n")) transistor_218 (.in(1'b0), .out(_321), .gate(H2));
  Transistor #(.\type ("n")) transistor_219 (.in(1'b0), .out(_302), .gate(not_7_out));
  Transistor #(.\type ("n")) transistor_220 (.in(1'b0), .out(_321), .gate(H1));
  Transistor #(.\type ("n")) transistor_221 (.in(1'b0), .out(_302), .gate(not_8_out));
  Transistor #(.\type ("n")) transistor_222 (.in(1'b0), .out(_302), .gate(H0));
  Transistor #(.\type ("n")) transistor_223 (.in(1'b0), .out(_321), .gate(not_9_out));
  Pull_Resistor #(.pull(1)) pull_resistor_33 (.node(_306));
  Transistor #(.\type ("n")) transistor_224 (.in(1'b0), .out(_306), .gate(not_1_out));
  Transistor #(.\type ("n")) transistor_225 (.in(1'b0), .out(_306), .gate(H7));
  Transistor #(.\type ("n")) transistor_226 (.in(1'b0), .out(_306), .gate(H6));
  Transistor #(.\type ("n")) transistor_227 (.in(1'b0), .out(_306), .gate(not_4_out));
  Transistor #(.\type ("n")) transistor_228 (.in(1'b0), .out(_306), .gate(not_5_out));
  Transistor #(.\type ("n")) transistor_229 (.in(1'b0), .out(_306), .gate(H3));
  Transistor #(.\type ("n")) transistor_230 (.in(1'b0), .out(_306), .gate(H2));
  Transistor #(.\type ("n")) transistor_231 (.in(1'b0), .out(_306), .gate(not_8_out));
  Transistor #(.\type ("n")) transistor_232 (.in(1'b0), .out(_306), .gate(H0));
  Pull_Resistor #(.pull(1)) pull_resistor_34 (.node(_340));
  Transistor #(.\type ("n")) transistor_233 (.in(1'b0), .out(_340), .gate(not_1_out));
  Transistor #(.\type ("n")) transistor_234 (.in(1'b0), .out(_340), .gate(H7));
  Transistor #(.\type ("n")) transistor_235 (.in(1'b0), .out(_340), .gate(not_3_out));
  Transistor #(.\type ("n")) transistor_236 (.in(1'b0), .out(_340), .gate(H5));
  Transistor #(.\type ("n")) transistor_237 (.in(1'b0), .out(_340), .gate(not_5_out));
  Transistor #(.\type ("n")) transistor_238 (.in(1'b0), .out(_340), .gate(H3));
  Transistor #(.\type ("n")) transistor_239 (.in(1'b0), .out(_340), .gate(not_7_out));
  Transistor #(.\type ("n")) transistor_240 (.in(1'b0), .out(_340), .gate(H1));
  Transistor #(.\type ("n")) transistor_241 (.in(1'b0), .out(_340), .gate(H0));

  assign Hnn = {H5, H4, H3, H2, H1, H0};
  assign VPOS = {V7, V6, V5, V4, V3, V2, V1, V0};

  // Notes on the sheet:
  //   H8
  //   H7
  //   H6
  //   H5
  //   H4
  //   H3
  //   H2
  //   H1
  //   H0
endmodule

module CONTROL_UNIT (
  input  PCLK,
  input  [5:0] Hnn,
  input  nOBCLIP,
  input  nBGCLIP,
  input  _65,
  input  _0_7__256_263,
  input  _0_255,
  input  _339,
  input  _63,
  input  _255,
  input  _0_63,
  input  _256_319,
  input  _0_255_2,
  input  _0_1,
  input  _2_3,
  input  _4_5,
  input  _6_7,
  input  _320_355,
  input  _0_255_3,
  input  _277,
  input  _302,
  input  _277_2,
  input  _256,
  input  _321,
  input  _306,
  input  _256_2,
  input  _4,
  input  _269,
  input  _272,
  input  _240,
  input  _1,
  input  _241,
  input  _0,
  input  _240_2,
  input  _311,
  input  _311_2,
  input  BLACK,
  input  _340,
  input  _265,
  output H0_prime_prime,
  output H1_prime_prime,
  output H2_prime_prime,
  output H3_prime_prime,
  output H4_prime_prime,
  output H5_prime_prime,
  output H0_prime,
  output H1_prime,
  output H2_prime,
  output S_EV,
  output CLIP_O,
  output CLIP_B,
  output _0_HPOS,
  output EVAL,
  output E_EV,
  output I_OAM2,
  output PAR_O,
  output nVIS,
  output F_NT,
  output F_AT,
  output F_TA,
  output F_TB,
  output nFO,
  output SC_CNT,
  output SYNC,
  output BURST,
  output PICTURE,
  output VSET,
  output VB,
  output BLNK,
  output VCLR,
  output VIN,
  output HC,
  output VC,
  output UNK_PAL_OAM_CTRL
);

  wire _1_out, _2_out, _5_out, and_1_out, and_2_out, and_3_out, and_4_out, d_latch_1_not_q, d_latch_2_q,
       d_latch_3_not_q, d_latch_4_not_q, d_latch_4_q, d_latch_5_q, d_latch_6_not_q, d_latch_6_q,
       d_latch_7_not_q, d_latch_8_not_q, d_latch_9_not_q, d_latch_10_not_q, d_latch_11_not_q,
       d_latch_12_not_q, d_latch_13_not_q, d_latch_14_q, d_latch_15_q, d_latch_16_not_q, d_latch_17_not_q,
       d_latch_18_not_q, d_latch_19_q, d_latch_20_q, d_latch_22_q, d_latch_23_q, d_latch_31_q, d_latch_32_q,
       d_latch_33_q, d_latch_34_q, d_latch_35_q, d_latch_36_q, d_latch_37_not_q, d_latch_39_not_q,
       d_latch_40_not_q, d_latch_41_not_q, d_latch_42_not_q, d_latch_43_not_q, d_latch_44_not_q,
       d_latch_45_not_q, d_latch_46_q, d_latch_54_q, d_latch_55_q, nor_1_out, nor_2_out, nor_3_out,
       nor_5_out, not_1_out, not_3_out, not_4_out, not_5_out, not_6_out, not_7_out, s_r_ff_1_q, s_r_ff_2_q,
       s_r_ff_3_q, s_r_ff_4_q, s_r_ff_5_q, s_r_ff_6_q, s_r_ff_7_q, s_r_ff_8_q;

  not not_1 (not_1_out, PCLK);
  D_latch d_latch_1 (.EN(not_1_out), .D(_65), .NOT_Q(d_latch_1_not_q));  // open: Q
  D_latch d_latch_2 (.EN(not_1_out), .D(_0_7__256_263), .Q(d_latch_2_q));  // open: NOT_Q
  D_latch d_latch_3 (.EN(not_1_out), .D(_0_255), .NOT_Q(d_latch_3_not_q));  // open: Q
  D_latch d_latch_4 (.EN(not_1_out), .D(_339), .Q(d_latch_4_q), .NOT_Q(d_latch_4_not_q));
  D_latch d_latch_5 (.EN(not_1_out), .D(_63), .Q(d_latch_5_q));  // open: NOT_Q
  D_latch d_latch_6 (.EN(not_1_out), .D(_255), .Q(d_latch_6_q), .NOT_Q(d_latch_6_not_q));
  D_latch d_latch_7 (.EN(not_1_out), .D(_0_63), .NOT_Q(d_latch_7_not_q));  // open: Q
  D_latch d_latch_8 (.EN(not_1_out), .D(_256_319), .NOT_Q(d_latch_8_not_q));  // open: Q
  D_latch d_latch_9 (.EN(not_1_out), .D(_0_255_2), .NOT_Q(d_latch_9_not_q));  // open: Q
  D_latch d_latch_10 (.EN(not_1_out), .D(_0_1), .NOT_Q(d_latch_10_not_q));  // open: Q
  D_latch d_latch_11 (.EN(not_1_out), .D(_2_3), .NOT_Q(d_latch_11_not_q));  // open: Q
  D_latch d_latch_12 (.EN(not_1_out), .D(_4_5), .NOT_Q(d_latch_12_not_q));  // open: Q
  D_latch d_latch_13 (.EN(not_1_out), .D(_6_7), .NOT_Q(d_latch_13_not_q));  // open: Q
  D_latch d_latch_14 (.EN(not_1_out), .D(_320_355), .Q(d_latch_14_q));  // open: NOT_Q
  D_latch d_latch_15 (.EN(not_1_out), .D(_0_255_3), .Q(d_latch_15_q));  // open: NOT_Q
  D_latch d_latch_16 (.EN(not_1_out), .D(_241), .NOT_Q(d_latch_16_not_q));  // open: Q
  D_latch d_latch_17 (.EN(not_1_out), .D(_311_2), .NOT_Q(d_latch_17_not_q));  // open: Q
  D_latch d_latch_18 (.EN(not_1_out), .D(_311_2), .NOT_Q(d_latch_18_not_q));  // open: Q
  D_latch d_latch_19 (.EN(not_1_out), .D(_311_2), .Q(d_latch_19_q));  // open: NOT_Q
  D_latch d_latch_20 (.EN(not_1_out), .D(_265), .Q(d_latch_20_q));  // open: NOT_Q
  nor nor_1 (nor_1_out, d_latch_2_q, d_latch_3_not_q);
  nor nor_2 (nor_2_out, d_latch_4_q, d_latch_5_q, d_latch_6_q);
  nor nor_3 (nor_3_out, d_latch_14_q, d_latch_15_q);
  S_R_Flip_Flop #(.trigger("high")) s_r_ff_1 (
    .S(_277), .clk(not_1_out), .R(_302), .Q(s_r_ff_1_q));  // open: Qn, preset, reset, en
  S_R_Flip_Flop #(.trigger("high")) s_r_ff_2 (
    .S(_277_2), .clk(not_1_out), .R(_256), .Q(s_r_ff_2_q));  // open: Qn, preset, reset, en
  S_R_Flip_Flop #(.trigger("high")) s_r_ff_3 (
    .S(_321), .clk(not_1_out), .R(_306), .Q(s_r_ff_3_q));  // open: Qn, preset, reset, en
  S_R_Flip_Flop #(.trigger("high")) s_r_ff_4 (
    .S(_256_2), .clk(not_1_out), .R(_4), .Q(s_r_ff_4_q));  // open: Qn, preset, reset, en
  not not_2 (VB, s_r_ff_5_q);
  S_R_Flip_Flop #(.trigger("high")) s_r_ff_5 (
    .S(_0), .clk(not_1_out), .R(_240_2), .Q(s_r_ff_5_q));  // open: Qn, preset, reset, en
  S_R_Flip_Flop #(.trigger("high")) s_r_ff_6 (
    .S(_240_2), .clk(not_1_out), .R(_311), .Q(s_r_ff_6_q));  // open: Qn, preset, reset, en
  nor _2 (_2_out, d_latch_19_q, _1_out);
  nor u__1 (_1_out, _2_out, d_latch_20_q);
  D_latch d_latch_21 (.EN(PCLK), .D(d_latch_1_not_q), .NOT_Q(S_EV));  // open: Q
  D_latch d_latch_22 (.EN(PCLK), .D(nor_1_out), .Q(d_latch_22_q));  // open: NOT_Q
  D_latch d_latch_23 (.EN(PCLK), .D(nor_1_out), .Q(d_latch_23_q));  // open: NOT_Q
  D_latch d_latch_24 (.EN(PCLK), .D(d_latch_4_not_q), .NOT_Q(_0_HPOS));  // open: Q
  D_latch d_latch_25 (.EN(PCLK), .D(nor_2_out), .Q(EVAL));  // open: NOT_Q
  D_latch d_latch_26 (.EN(PCLK), .D(d_latch_6_not_q), .NOT_Q(E_EV));  // open: Q
  D_latch d_latch_27 (.EN(PCLK), .D(d_latch_7_not_q), .NOT_Q(I_OAM2));  // open: Q
  D_latch d_latch_28 (.EN(PCLK), .D(d_latch_8_not_q), .NOT_Q(PAR_O));  // open: Q
  D_latch d_latch_29 (.EN(PCLK), .D(d_latch_9_not_q), .Q(nVIS));  // open: NOT_Q
  D_latch d_latch_30 (.EN(PCLK), .D(d_latch_10_not_q), .NOT_Q(F_NT));  // open: Q
  D_latch d_latch_31 (.EN(PCLK), .D(d_latch_12_not_q), .Q(d_latch_31_q));  // open: NOT_Q
  D_latch d_latch_32 (.EN(PCLK), .D(d_latch_13_not_q), .Q(d_latch_32_q));  // open: NOT_Q
  D_latch d_latch_33 (.EN(PCLK), .D(nor_3_out), .Q(d_latch_33_q), .NOT_Q(nFO));
  D_latch d_latch_34 (.EN(PCLK), .D(not_3_out), .Q(d_latch_34_q));  // open: NOT_Q
  not not_3 (not_3_out, s_r_ff_2_q);
  D_latch d_latch_35 (.EN(PCLK), .D(s_r_ff_3_q), .Q(d_latch_35_q));  // open: NOT_Q
  D_latch d_latch_36 (.EN(PCLK), .D(nor_5_out), .Q(d_latch_36_q));  // open: NOT_Q
  D_latch d_latch_37 (.EN(PCLK), .D(d_latch_16_not_q), .NOT_Q(d_latch_37_not_q));  // open: Q
  D_latch d_latch_38 (.EN(PCLK), .D(d_latch_17_not_q), .NOT_Q(VCLR));  // open: Q
  D_latch d_latch_39 (.EN(PCLK), .D(_1_out), .NOT_Q(d_latch_39_not_q));  // open: Q
  D_latch d_latch_40 (.EN(not_1_out), .D(Hnn[0]), .Q(H0_prime), .NOT_Q(d_latch_40_not_q));
  D_latch d_latch_41 (.EN(not_1_out), .D(Hnn[1]), .Q(H1_prime), .NOT_Q(d_latch_41_not_q));
  D_latch d_latch_42 (.EN(not_1_out), .D(Hnn[2]), .Q(H2_prime), .NOT_Q(d_latch_42_not_q));
  D_latch d_latch_43 (.EN(not_1_out), .D(Hnn[3]), .NOT_Q(d_latch_43_not_q));  // open: Q
  D_latch d_latch_44 (.EN(not_1_out), .D(Hnn[4]), .NOT_Q(d_latch_44_not_q));  // open: Q
  D_latch d_latch_45 (.EN(not_1_out), .D(Hnn[5]), .NOT_Q(d_latch_45_not_q));  // open: Q
  nor nor_4 (SYNC, d_latch_34_q, d_latch_36_q);
  nor nor_5 (nor_5_out, s_r_ff_1_q, s_r_ff_7_q);
  and and_1 (and_1_out, s_r_ff_1_q, _269);
  and and_2 (and_2_out, s_r_ff_1_q, _272);
  and and_3 (and_3_out, s_r_ff_4_q, _240);
  and and_4 (and_4_out, s_r_ff_4_q, _1);
  nand _5 (_5_out, BLNK, d_latch_39_not_q);
  S_R_Flip_Flop #(.trigger("high")) s_r_ff_7 (
    .S(and_1_out), .clk(1'b1), .R(and_2_out), .Q(s_r_ff_7_q));  // open: Qn, preset, reset, en
  S_R_Flip_Flop #(.trigger("high")) s_r_ff_8 (
    .S(and_3_out), .clk(1'b1), .R(and_4_out), .Q(s_r_ff_8_q));  // open: Qn, preset, reset, en
  D_latch d_latch_46 (.EN(not_1_out), .D(d_latch_37_not_q), .Q(d_latch_46_q));  // open: NOT_Q
  not not_4 (not_4_out, _340);
  not not_5 (not_5_out, H0_prime);
  nor nor_6 (VSET, not_1_out, d_latch_46_q, d_latch_16_not_q);
  D_latch d_latch_47 (.EN(not_1_out), .D(not_4_out), .NOT_Q(HC));  // open: Q
  nor _6 (UNK_PAL_OAM_CTRL, not_1_out, _5_out, not_5_out);
  D_latch d_latch_48 (.EN(PCLK), .D(d_latch_40_not_q), .NOT_Q(H0_prime_prime));  // open: Q
  D_latch d_latch_49 (.EN(PCLK), .D(d_latch_41_not_q), .NOT_Q(H1_prime_prime));  // open: Q
  D_latch d_latch_50 (.EN(PCLK), .D(d_latch_42_not_q), .NOT_Q(H2_prime_prime));  // open: Q
  D_latch d_latch_51 (.EN(PCLK), .D(d_latch_43_not_q), .NOT_Q(H3_prime_prime));  // open: Q
  D_latch d_latch_52 (.EN(PCLK), .D(d_latch_44_not_q), .NOT_Q(H4_prime_prime));  // open: Q
  D_latch d_latch_53 (.EN(PCLK), .D(d_latch_45_not_q), .NOT_Q(H5_prime_prime));  // open: Q
  nor nor_7 (CLIP_O, d_latch_22_q, nOBCLIP);
  nor nor_8 (CLIP_B, d_latch_23_q, nBGCLIP);
  nor nor_9 (F_AT, d_latch_11_not_q, nor_3_out);
  nor nor_10 (F_TA, d_latch_31_q, d_latch_33_q);
  nor nor_11 (F_TB, d_latch_33_q, d_latch_32_q);
  not not_6 (not_6_out, s_r_ff_1_q);
  or or_1 (BLNK, s_r_ff_6_q, BLACK);
  nor nor_12 (SC_CNT, not_6_out, BLACK);
  nor nor_13 (BURST, SYNC, d_latch_35_q);
  or or_2 (PICTURE, d_latch_54_q, d_latch_55_q);
  D_latch d_latch_54 (.EN(s_r_ff_4_q), .Q(d_latch_54_q));  // open: D, NOT_Q
  D_latch d_latch_55 (.EN(s_r_ff_4_q), .D(s_r_ff_8_q), .Q(d_latch_55_q));  // open: NOT_Q
  not not_7 (not_7_out, HC);
  nor _12 (VC, not_7_out, d_latch_18_not_q);

  assign VIN = _340;

  // Notes on the sheet:
  //   VPOS control
  //   VPLA8
  //   H/V control
  //   HPLA 23
  //   VPLA 9 
  //   HPOS control
  //   Front porch RS flip/flop
  //   Back porch flip/flop
  //   7
  //   2
  //   1
  //   /FPORCH
  //   BPORCH
  //   /VSET
  //   BPORCH
  //   3
  //   /HB
  //   VSYNC
  //   /HB
  //   9
  //   10
  //   4
  //   BLACK
  //   11
endmodule

module REGISTER_SELECT (
  input  nDBE,
  input  RC,
  input  RS0,
  input  RS1,
  input  RS2,
  input  R_W,
  output nW6_1,
  output nW6_2,
  output nW5_1,
  output nW5_2,
  output nR7,
  output nW7,
  output nW4,
  output nW3,
  output nR2,
  output nW1,
  output nW0,
  output nR4
);

  wire multiplexer_1_out, multiplexer_2_out, nor_1_out, nor_2_out, nor_3_out, nor_4_out, nor_5_out,
       nor_6_out, nor_7_out, nor_8_out, nor_9_out, nor_10_out, nor_11_out, nor_12_out, nor_13_out,
       nor_14_out, nor_15_out, nor_16_out, nor_17_out, not_1_out, not_2_out, not_3_out, not_4_out, not_5_out,
       not_6_out;

  not not_1 (not_1_out, RS0);
  not not_2 (not_2_out, RS1);
  not not_3 (not_3_out, RS2);
  not not_4 (not_4_out, R_W);
  nor nor_1 (nor_1_out, nor_16_out, RC, multiplexer_1_out);
  Multiplexer #(.enable("false")) multiplexer_1 (
    .in0(not_6_out), .in1(not_5_out), .out(multiplexer_1_out), .sel(nor_15_out));
  not not_5 (not_5_out, nor_1_out);
  Multiplexer #(.enable("false")) multiplexer_2 (
    .in0(not_6_out), .in1(nor_1_out), .out(multiplexer_2_out), .sel(nor_15_out));
  nor nor_2 (nor_2_out, nor_16_out, RC, multiplexer_2_out);
  not not_6 (not_6_out, nor_2_out);
  nor nor_3 (nor_3_out, RS0, not_2_out, not_3_out, R_W, nor_1_out);
  nor nor_4 (nor_4_out, RS0, not_2_out, not_3_out, R_W, not_5_out);
  nor nor_5 (nor_5_out, not_1_out, RS1, not_3_out, R_W, nor_1_out);
  nor nor_6 (nor_6_out, not_1_out, RS1, not_3_out, R_W, not_5_out);
  not not_7 (nR7, nor_7_out);
  nor nor_7 (nor_7_out, not_1_out, not_2_out, not_3_out, not_4_out);
  nor nor_8 (nor_8_out, not_1_out, not_2_out, not_3_out, R_W);
  not not_8 (nW7, nor_8_out);
  not not_9 (nW4, nor_9_out);
  nor nor_9 (nor_9_out, RS0, RS1, not_3_out, R_W);
  nor nor_10 (nor_10_out, not_1_out, not_2_out, RS2, R_W);
  not not_10 (nW3, nor_10_out);
  not not_11 (nR2, nor_11_out);
  nor nor_11 (nor_11_out, RS0, not_2_out, RS2, not_4_out);
  not not_12 (nW1, nor_12_out);
  nor nor_12 (nor_12_out, not_1_out, RS1, RS2, R_W);
  not not_13 (nW0, nor_13_out);
  nor nor_13 (nor_13_out, RS0, RS1, RS2, R_W);
  nor nor_14 (nor_14_out, RS0, RS1, not_3_out, not_4_out);
  not not_14 (nR4, nor_14_out);
  nor nor_15 (nor_15_out, nDBE, nor_17_out);
  nor nor_16 (nor_16_out, nDBE, nR2);
  nor nor_17 (nor_17_out, nor_3_out, nor_4_out, nor_5_out, nor_6_out);
  not not_15 (nW6_1, nor_3_out);
  not not_16 (nW6_2, nor_4_out);
  not not_17 (nW5_1, nor_5_out);
  not not_18 (nW5_2, nor_6_out);

  // Notes on the sheet:
  //   1ST
  //   2ND
  //   $2005/$2006 first/second write latch
  //   W5/6
  //   R2
endmodule

module VIDEO_OUT (
  input  CLK,
  input  RES,
  input  nTR,
  input  nTG,
  input  nTB,
  input  V0,
  input  PCLK,
  input  nCC0,
  input  nCC1,
  input  nCC2,
  input  nCC3,
  input  PICTURE,
  input  SYNC,
  input  BURST,
  input  nLL0,
  input  nLL1,
  output [10:0] out_17
);

  wire _1_out, _2_out, _3_out, _4_out, _5_out, _6_out, _7_out, _8_out, _9_out, _10_out, _11_out, _12_out,
       _13_out, _14_out, _15_out, _16_2_out, _16_out, _17_out, _18_out, _19_out, _20_out, _21_out, _22_out,
       _23_out, _24_2_out, _24_out, _25_out, _31_out, _32_out, _33_out, _34_out, _42_out, _44_out,
       d_latch_1_not_q, d_latch_2_not_q, d_latch_3_not_q, d_latch_4_not_q, d_latch_5_not_q, d_latch_6_not_q,
       d_latch_7_not_q, d_latch_8_not_q, d_latch_9_not_q, d_latch_10_q, d_latch_11_q, d_latch_12_q,
       d_latch_13_not_q, d_latch_14_not_q, d_latch_15_not_q, d_latch_16_not_q, d_latch_17_q, d_latch_18_q,
       d_latch_19_q, d_latch_20_not_q, d_latch_21_q, d_latch_22_not_q, d_latch_23_q, d_latch_24_not_q,
       d_latch_25_q, d_latch_26_not_q, d_latch_27_q, d_latch_28_not_q, multiplexer_1_out, multiplexer_2_out,
       nor_1_out, nor_2_out, nor_3_out, nor_4_out, nor_5_out, nor_6_out, nor_7_out, nor_8_out, nor_9_out,
       nor_10_out, nor_11_out, nor_12_out, nor_13_out, nor_14_out, nor_15_out, nor_16_out, nor_17_out,
       nor_18_out, nor_19_out, nor_20_out, nor_21_out, nor_22_out, nor_23_out, not_1_out, not_2_out,
       not_3_out, not_4_out, not_5_out, not_6_out, not_7_out, not_8_out, not_9_out, not_10_out, not_11_out,
       not_12_out, not_13_out, not_14_out, not_15_out, not_16_out, not_17_out, not_18_out, not_20_out,
       not_26_out, not_27_out, not_30_out, not_31_out;

  not not_1 (not_1_out, PICTURE);
  not not_2 (not_2_out, PCLK);
  D_latch d_latch_1 (.EN(PCLK), .D(nCC0), .NOT_Q(d_latch_1_not_q));  // open: Q
  D_latch d_latch_2 (.EN(PCLK), .D(nCC1), .NOT_Q(d_latch_2_not_q));  // open: Q
  D_latch d_latch_3 (.EN(PCLK), .D(nCC2), .NOT_Q(d_latch_3_not_q));  // open: Q
  D_latch d_latch_4 (.EN(PCLK), .D(nCC3), .NOT_Q(d_latch_4_not_q));  // open: Q
  D_latch d_latch_5 (.EN(not_2_out), .D(not_1_out), .NOT_Q(d_latch_5_not_q));  // open: Q
  or _42 (_42_out, _44_out, SYNC, BURST);
  not not_3 (not_3_out, SYNC);
  nor _31 (_31_out, not_6_out, nTR, d_latch_13_not_q);
  nor _32 (_32_out, d_latch_13_not_q, nTG, not_7_out);
  nor _33 (_33_out, d_latch_13_not_q, nTB, nor_15_out);
  D_latch d_latch_6 (.EN(not_2_out), .D(V0), .NOT_Q(d_latch_6_not_q));  // open: Q
  D_latch d_latch_7 (.EN(not_2_out), .D(d_latch_1_not_q), .NOT_Q(d_latch_7_not_q));  // open: Q
  D_latch d_latch_8 (.EN(not_2_out), .D(d_latch_2_not_q), .NOT_Q(d_latch_8_not_q));  // open: Q
  D_latch d_latch_9 (.EN(not_2_out), .D(d_latch_3_not_q), .NOT_Q(d_latch_9_not_q));  // open: Q
  D_latch d_latch_10 (.EN(not_2_out), .D(d_latch_4_not_q), .Q(d_latch_10_q));  // open: NOT_Q
  D_latch d_latch_11 (.EN(PCLK), .D(d_latch_5_not_q), .Q(d_latch_11_q));  // open: NOT_Q
  D_latch d_latch_12 (.EN(not_2_out), .D(_42_out), .Q(d_latch_12_q));  // open: NOT_Q
  D_latch d_latch_13 (.EN(not_2_out), .D(_44_out), .NOT_Q(d_latch_13_not_q));  // open: Q
  D_latch d_latch_14 (.EN(not_2_out), .D(_42_out), .NOT_Q(d_latch_14_not_q));  // open: Q
  D_latch d_latch_15 (.EN(not_2_out), .D(not_3_out), .NOT_Q(d_latch_15_not_q));  // open: Q
  D_latch d_latch_16 (.EN(not_2_out), .D(BURST), .NOT_Q(d_latch_16_not_q));  // open: Q
  nor _34 (_34_out, _31_out, _32_out, _33_out);
  not not_4 (not_4_out, _34_out);
  nor nor_1 (nor_1_out, d_latch_10_q, d_latch_12_q);
  nor _44 (_44_out, d_latch_11_q, _24_out);
  not not_5 (not_5_out, nLL0);
  not not_6 (not_6_out, multiplexer_1_out);
  not not_7 (not_7_out, multiplexer_2_out);
  nor _24 (_24_out, nor_1_out, d_latch_9_not_q, d_latch_8_not_q);
  not not_8 (not_8_out, nLL1);
  Multiplexer #(.enable("false")) multiplexer_1 (
    .in0(nor_18_out), .in1(nor_10_out), .out(multiplexer_1_out), .sel(d_latch_6_not_q));
  Multiplexer #(.enable("false")) multiplexer_2 (
    .in0(nor_10_out), .in1(nor_18_out), .out(multiplexer_2_out), .sel(d_latch_6_not_q));
  nor nor_2 (nor_2_out, d_latch_13_not_q, not_5_out, not_8_out);
  nor nor_3 (nor_3_out, d_latch_13_not_q, nLL0, nLL1);
  nor nor_4 (nor_4_out, d_latch_13_not_q, nLL0, not_8_out);
  nor nor_5 (nor_5_out, d_latch_13_not_q, not_5_out, nLL1);
  not not_9 (not_9_out, d_latch_6_not_q);
  not not_10 (not_10_out, d_latch_7_not_q);
  not not_11 (not_11_out, d_latch_8_not_q);
  not not_12 (not_12_out, d_latch_9_not_q);
  not not_13 (not_13_out, nor_1_out);
  nor _1 (_1_out, d_latch_6_not_q, d_latch_7_not_q, not_11_out, d_latch_9_not_q, not_13_out, nor_6_out);
  not not_14 (not_14_out, nor_2_out);
  not not_15 (not_15_out, nor_3_out);
  not not_16 (not_16_out, nor_4_out);
  not not_17 (not_17_out, nor_5_out);
  not not_18 (not_18_out, CLK);
  nor _2 (_2_out, not_9_out, not_10_out, not_11_out, d_latch_9_not_q, nor_1_out, nor_6_out);
  D_latch d_latch_17 (.EN(not_18_out), .D(not_26_out), .Q(d_latch_17_q));  // open: NOT_Q
  not not_19 (out_17[0], not_4_out);
  not not_20 (not_20_out, d_latch_14_not_q);
  not not_21 (out_17[10], d_latch_15_not_q);
  nor nor_6 (nor_6_out, RES, d_latch_17_q);
  nor _3 (_3_out, d_latch_6_not_q, not_10_out, not_11_out, d_latch_9_not_q, nor_1_out, nor_9_out);
  nor nor_7 (nor_7_out, nor_19_out, d_latch_16_not_q);
  nor nor_8 (nor_8_out, nor_7_out, d_latch_16_not_q);
  D_latch d_latch_18 (.EN(CLK), .D(nor_6_out), .Q(d_latch_18_q));  // open: NOT_Q
  nor _16 (_16_out, not_26_out, d_latch_20_not_q);
  nor _4 (_4_out, not_9_out, d_latch_7_not_q, not_11_out, d_latch_9_not_q, not_13_out, nor_9_out);
  not not_22 (out_17[6], nor_7_out);
  not not_23 (out_17[9], nor_8_out);
  nor nor_9 (nor_9_out, d_latch_18_q, _16_out);
  nor _5 (_5_out, d_latch_6_not_q, d_latch_7_not_q, d_latch_8_not_q, d_latch_9_not_q, not_13_out, nor_10_out);
  or or_1 (out_17[7], not_20_out, not_30_out);
  D_latch d_latch_19 (.EN(not_18_out), .D(nor_9_out), .Q(d_latch_19_q));  // open: NOT_Q
  nor _6 (_6_out, not_9_out, not_10_out, d_latch_8_not_q, not_12_out, nor_1_out, nor_10_out);
  nor nor_10 (nor_10_out, RES, d_latch_19_q);
  nor _7 (_7_out, d_latch_6_not_q, not_10_out, d_latch_8_not_q, not_12_out, not_13_out, d_latch_20_not_q);
  nor nor_11 (nor_11_out, nor_19_out, not_14_out);
  not not_24 (out_17[4], nor_11_out);
  not not_25 (out_17[8], nor_12_out);
  nor nor_12 (nor_12_out, nor_11_out, not_14_out);
  D_latch d_latch_20 (.EN(CLK), .D(nor_10_out), .NOT_Q(d_latch_20_not_q));  // open: Q
  nor _8 (_8_out, not_9_out, d_latch_7_not_q, d_latch_8_not_q, not_12_out, not_13_out, d_latch_20_not_q);
  D_latch d_latch_21 (.EN(not_18_out), .D(d_latch_20_not_q), .Q(d_latch_21_q));  // open: NOT_Q
  nor _9 (_9_out, d_latch_6_not_q, d_latch_7_not_q, not_11_out, not_12_out, nor_1_out, nor_15_out);
  nor nor_13 (nor_13_out, nor_19_out, not_15_out);
  nor nor_14 (nor_14_out, nor_13_out, not_15_out);
  nor nor_15 (nor_15_out, RES, d_latch_21_q);
  not not_26 (not_26_out, d_latch_22_not_q);
  nor _10 (_10_out, not_9_out, not_10_out, not_11_out, not_12_out, nor_1_out, nor_15_out);
  not not_27 (not_27_out, nor_13_out);
  not not_28 (out_17[2], nor_14_out);
  or or_2 (out_17[1], not_27_out, not_31_out);
  D_latch d_latch_22 (.EN(CLK), .D(nor_15_out), .NOT_Q(d_latch_22_not_q));  // open: Q
  D_latch d_latch_23 (.EN(not_18_out), .D(d_latch_22_not_q), .Q(d_latch_23_q));  // open: NOT_Q
  nor _11 (_11_out, not_10_out, not_11_out, not_12_out, not_13_out);
  nor nor_16 (nor_16_out, nor_19_out, not_16_out);
  nor nor_17 (nor_17_out, nor_16_out, not_16_out);
  nor nor_18 (nor_18_out, RES, d_latch_23_q);
  nor _12 (_12_out, d_latch_6_not_q, not_10_out, not_11_out, d_latch_9_not_q, not_13_out, d_latch_22_not_q);
  not not_29 (out_17[3], nor_16_out);
  not not_30 (not_30_out, nor_17_out);
  D_latch d_latch_24 (.EN(CLK), .D(nor_18_out), .NOT_Q(d_latch_24_not_q));  // open: Q
  nor _13 (_13_out, not_9_out, d_latch_7_not_q, not_11_out, not_12_out, not_13_out, d_latch_22_not_q);
  nor nor_19 (nor_19_out, _1_out, _2_out, _3_out, _4_out, _5_out, _6_out, _7_out, _8_out, _9_out, _10_out, _11_out, _12_out, _13_out, _14_out, _15_out, _16_2_out, _17_out, _18_out, _19_out, _20_out, _21_out, _22_out, _23_out, _24_2_out, _25_out);
  nor nor_20 (nor_20_out, nor_19_out, not_17_out);
  nor nor_21 (nor_21_out, nor_20_out, not_17_out);
  D_latch d_latch_25 (.EN(not_18_out), .D(d_latch_24_not_q), .Q(d_latch_25_q));  // open: NOT_Q
  nor _14 (_14_out, d_latch_6_not_q, d_latch_7_not_q, d_latch_8_not_q, not_12_out, nor_1_out, nor_18_out);
  not not_31 (not_31_out, nor_20_out);
  not not_32 (out_17[5], nor_21_out);
  nor nor_22 (nor_22_out, RES, d_latch_25_q);
  D_latch d_latch_26 (.EN(CLK), .D(nor_22_out), .NOT_Q(d_latch_26_not_q));  // open: Q
  nor _15 (_15_out, not_9_out, not_10_out, d_latch_8_not_q, d_latch_9_not_q, not_13_out, nor_18_out);
  D_latch d_latch_27 (.EN(not_18_out), .D(d_latch_26_not_q), .Q(d_latch_27_q));  // open: NOT_Q
  nor _16_2 (_16_2_out, d_latch_6_not_q, not_10_out, d_latch_8_not_q, d_latch_9_not_q, not_13_out, d_latch_24_not_q);
  nor nor_23 (nor_23_out, RES, d_latch_27_q);
  nor _17 (_17_out, not_9_out, d_latch_7_not_q, d_latch_8_not_q, not_12_out, nor_1_out, d_latch_24_not_q);
  D_latch d_latch_28 (.EN(CLK), .D(nor_23_out), .NOT_Q(d_latch_28_not_q));  // open: Q
  nor _18 (_18_out, d_latch_6_not_q, d_latch_7_not_q, not_11_out, not_12_out, not_13_out, nor_22_out);
  nor _19 (_19_out, not_9_out, not_10_out, not_11_out, d_latch_9_not_q, not_13_out, nor_22_out);
  nor _20 (_20_out, d_latch_6_not_q, not_10_out, not_11_out, not_12_out, nor_1_out, d_latch_26_not_q);
  nor _21 (_21_out, not_9_out, d_latch_7_not_q, not_11_out, not_12_out, nor_1_out, d_latch_26_not_q);
  nor _22 (_22_out, d_latch_6_not_q, d_latch_7_not_q, d_latch_8_not_q, not_12_out, not_13_out, nor_23_out);
  nor _23 (_23_out, not_9_out, not_10_out, d_latch_8_not_q, not_12_out, not_13_out, nor_23_out);
  nor _24_2 (_24_2_out, d_latch_6_not_q, not_10_out, d_latch_8_not_q, not_12_out, nor_1_out, d_latch_28_not_q);
  nor _25 (_25_out, not_9_out, d_latch_7_not_q, d_latch_8_not_q, d_latch_9_not_q, not_13_out, d_latch_28_not_q);

  // Notes on the sheet:
  //   Emphasis
  //   50
  //   !
  //   51
  //   !
  //   41
  //   52
  //   !
  //   45
  //   47
  //   46
  //   48
  //   /PR
  //   /PG
  //   35
  //   /POUT
  //   14
  //   13
  //   TINT
  //   /PB
  //   /POUT
  //   P123
  //   /V0'
  //   0
  //   1
  //   2
  //   3
  //   /POUT
  //   /LU3
  //   /LU0
  //   /LU2
  //   /LU1
  //   49
  //   TINT
  //   Color 1D (black)
  //   Synch
  //   Color burst
  //   1
  //   /PZ
  //   2
  //   3
  //   4
  //   5
  //   6
  //   15
  //   7
  //   /V0
  //   0
  //   1
  //   2
  //   3
  //   8
  //   9
  //   /PZ
  //   10
  //   11
  //   12
  //   /V0
  //   0
  //   1
  //   2
  //   3
endmodule

module RW_CONTROL (
  input  R_W,
  input  nDBE,
  output nRD,
  output nWR
);

  wire nor_1_out, nor_2_out, not_1_out;

  not not_1 (not_1_out, R_W);
  nor nor_1 (nor_1_out, not_1_out, nDBE);
  nor nor_2 (nor_2_out, R_W, nDBE);
  not not_2 (nRD, nor_1_out);
  not not_3 (nWR, nor_2_out);

  // Notes on the sheet:
  //   R/W = 0: write data to PPU
  //   /RD = 0: CPU read data from PPU
  //   /WR = 0: CPU write data to PPU
endmodule

module CPU_DATA_PAD (
  input  nRD,
  input  nWR,
  input  PPU_CPU,
  input  PPU_data_in,
  output PPU_ADRESS_OUT,
  output CPU_PPU
);

  wire not_1_out, not_2_out;

  not not_1 (not_1_out, nRD);
  not not_2 (not_2_out, nWR);
  assign PPU_ADRESS_OUT = not_1_out ? PPU_CPU : 1'bz;  // Controlled_Buffer controlled_buffer_1
  assign CPU_PPU = not_2_out ? PPU_data_in : 1'bz;  // Controlled_Buffer controlled_buffer_2

  // Notes on the sheet:
  //   /RD = 0: CPU read data from PPU
  //   /WR = 0: CPU write data to PPU
endmodule

module INTERRUPT_CONTROL (
  input  VBL_EN,
  input  VSET,
  input  VCLR,
  input  nDBE,
  input  nR2,
  output INT,
  output DB7
);

  wire d_latch_1_q, nor_1_out, not_1_out, or_1_out, s_r_ff_1_q;

  nor nor_1 (nor_1_out, nDBE, nR2);
  or or_1 (or_1_out, VCLR, nor_1_out);
  not not_1 (not_1_out, nor_1_out);
  S_R_Flip_Flop #(.trigger("high")) s_r_ff_1 (
    .S(VSET), .clk(1'b1), .R(or_1_out), .Q(s_r_ff_1_q));  // open: Qn, preset, reset, en
  and and_1 (INT, VBL_EN, s_r_ff_1_q);
  D_latch d_latch_1 (.EN(not_1_out), .D(s_r_ff_1_q), .Q(d_latch_1_q));  // open: NOT_Q
  Multiplexer multiplexer_1 (.in0(1'b0), .in1(1'b1), .out(DB7), .sel(d_latch_1_q), .en(nor_1_out));

  // Notes on the sheet:
  //   R2_EN
  //   VBLANK FLIP/FLOP
  //   TRI-STATE
endmodule

module COLOR_BUFFER_BIT (
  input  PCLK,
  input  CB_DB,
  input  RAM_CB,
  input  OE,
  input  DB_CB,
  input  DB,
  output DB_2,
  output nout,
  output CB_RAM
);

  wire and_1_out, d_latch_1_not_q, d_latch_2_q, d_latch_3_not_q, nand_1_out, nor_1_out, nor_2_out, not_1_out,
       not_2_out;

  not not_1 (not_1_out, PCLK);
  not not_2 (not_2_out, PCLK);
  D_latch d_latch_1 (.EN(not_1_out), .D(nout), .NOT_Q(d_latch_1_not_q));  // open: Q
  D_latch d_latch_2 (.EN(PCLK), .D(1'b1), .Q(d_latch_2_q));  // open: NOT_Q
  and and_1 (and_1_out, not_2_out, nor_2_out);
  D_latch d_latch_3 (.EN(PCLK), .D(d_latch_1_not_q), .NOT_Q(d_latch_3_not_q));  // open: Q
  nor nor_1 (nor_1_out, d_latch_2_q, and_1_out);
  nor nor_2 (nor_2_out, nor_1_out, RAM_CB);
  assign CB_RAM = DB_CB ? DB : 1'bz;  // Controlled_Buffer controlled_buffer_1
  assign DB_2 = CB_DB ? d_latch_3_not_q : 1'bz;  // Controlled_Buffer controlled_buffer_2
  nand nand_1 (nand_1_out, nor_2_out, OE);
  not not_3 (nout, nand_1_out);
endmodule
module COLOR_RAM (
  input  PAL2,
  input  PAL3,
  input  PAL4,
  input  PAL0,
  input  PAL1,
  input  PCLK,
  input  CB3_RAM,
  input  CB2_RAM,
  input  CB1_RAM,
  input  CB0_RAM,
  input  CY1_RAM,
  input  CY0_RAM,
  output RAM_CB3,
  output RAM_CY0,
  output RAM_CB2,
  output RAM_CB1,
  output RAM_CB0,
  output RAM_CY1
);

  wire and_1_out, and_2_out, and_3_out, and_4_out, and_5_out, and_6_out, and_7_out, controlled_buffer_1_out,
       controlled_buffer_2_out, controlled_buffer_3_out, controlled_buffer_4_out, controlled_buffer_5_out,
       controlled_buffer_6_out, controlled_buffer_7_out, controlled_buffer_8_out, controlled_buffer_9_out,
       controlled_buffer_16_out, controlled_buffer_17_out, controlled_buffer_18_out,
       controlled_buffer_19_out, controlled_buffer_20_out, controlled_buffer_21_out,
       controlled_buffer_22_out, controlled_buffer_23_out, controlled_buffer_24_out,
       controlled_buffer_25_out, controlled_buffer_32_out, controlled_buffer_34_out,
       controlled_buffer_35_out, controlled_buffer_36_out, controlled_buffer_37_out,
       controlled_buffer_38_out, controlled_buffer_39_out, controlled_buffer_40_out,
       controlled_buffer_41_out, controlled_buffer_42_out, controlled_buffer_44_out,
       controlled_buffer_46_out, controlled_buffer_48_out, controlled_buffer_50_out,
       controlled_buffer_52_out, controlled_buffer_54_out, controlled_buffer_56_out,
       controlled_buffer_57_out, controlled_buffer_65_out, controlled_buffer_66_out,
       controlled_buffer_67_out, controlled_buffer_68_out, controlled_buffer_69_out,
       controlled_buffer_70_out, controlled_buffer_71_out, controlled_buffer_72_out,
       controlled_buffer_73_out, controlled_buffer_80_out, controlled_buffer_81_out,
       controlled_buffer_82_out, controlled_buffer_83_out, controlled_buffer_84_out,
       controlled_buffer_85_out, controlled_buffer_86_out, controlled_buffer_87_out,
       controlled_buffer_88_out, controlled_buffer_89_out, controlled_buffer_96_out,
       controlled_buffer_98_out, controlled_buffer_99_out, controlled_buffer_100_out,
       controlled_buffer_101_out, controlled_buffer_102_out, controlled_buffer_103_out,
       controlled_buffer_104_out, controlled_buffer_105_out, controlled_buffer_106_out,
       controlled_buffer_108_out, controlled_buffer_110_out, controlled_buffer_112_out,
       controlled_buffer_114_out, controlled_buffer_116_out, controlled_buffer_118_out,
       controlled_buffer_120_out, controlled_buffer_121_out, controlled_buffer_129_out,
       controlled_buffer_130_out, controlled_buffer_131_out, controlled_buffer_132_out,
       controlled_buffer_133_out, controlled_buffer_134_out, controlled_buffer_135_out,
       controlled_buffer_136_out, controlled_buffer_137_out, controlled_buffer_144_out,
       controlled_buffer_145_out, controlled_buffer_146_out, controlled_buffer_147_out,
       controlled_buffer_148_out, controlled_buffer_149_out, controlled_buffer_150_out,
       controlled_buffer_151_out, controlled_buffer_152_out, controlled_buffer_153_out,
       controlled_buffer_160_out, controlled_buffer_162_out, controlled_buffer_163_out,
       controlled_buffer_164_out, controlled_buffer_165_out, controlled_buffer_166_out,
       controlled_buffer_167_out, controlled_buffer_168_out, controlled_buffer_169_out,
       controlled_buffer_170_out, controlled_buffer_172_out, controlled_buffer_174_out,
       controlled_buffer_176_out, controlled_buffer_178_out, controlled_buffer_180_out,
       controlled_buffer_182_out, controlled_buffer_184_out, controlled_buffer_185_out,
       controlled_buffer_193_out, controlled_buffer_194_out, controlled_buffer_195_out,
       controlled_buffer_196_out, controlled_buffer_197_out, controlled_buffer_198_out,
       controlled_buffer_199_out, controlled_buffer_200_out, controlled_buffer_201_out,
       controlled_buffer_208_out, controlled_buffer_209_out, controlled_buffer_210_out,
       controlled_buffer_211_out, controlled_buffer_212_out, controlled_buffer_213_out,
       controlled_buffer_214_out, controlled_buffer_215_out, controlled_buffer_216_out,
       controlled_buffer_217_out, controlled_buffer_218_out, controlled_buffer_220_out,
       controlled_buffer_222_out, controlled_buffer_224_out, controlled_buffer_226_out,
       controlled_buffer_228_out, controlled_buffer_230_out, controlled_buffer_231_out,
       controlled_buffer_233_out, controlled_buffer_234_out, controlled_buffer_236_out,
       controlled_buffer_238_out, controlled_buffer_240_out, controlled_buffer_242_out,
       controlled_buffer_244_out, controlled_buffer_246_out, controlled_buffer_248_out,
       controlled_buffer_249_out, controlled_buffer_257_out, controlled_buffer_258_out,
       controlled_buffer_259_out, controlled_buffer_260_out, controlled_buffer_261_out,
       controlled_buffer_262_out, controlled_buffer_263_out, controlled_buffer_264_out,
       controlled_buffer_265_out, controlled_buffer_266_out, controlled_buffer_268_out,
       controlled_buffer_270_out, controlled_buffer_272_out, controlled_buffer_274_out,
       controlled_buffer_276_out, controlled_buffer_278_out, controlled_buffer_279_out,
       controlled_buffer_280_out, controlled_buffer_281_out, controlled_buffer_282_out,
       controlled_buffer_284_out, controlled_buffer_286_out, controlled_buffer_288_out,
       controlled_buffer_290_out, controlled_buffer_292_out, controlled_buffer_294_out,
       controlled_buffer_295_out, controlled_buffer_297_out, controlled_buffer_305_out,
       controlled_buffer_306_out, controlled_buffer_307_out, controlled_buffer_308_out,
       controlled_buffer_309_out, controlled_buffer_310_out, controlled_buffer_311_out,
       controlled_buffer_312_out, controlled_buffer_313_out, controlled_buffer_321_out,
       controlled_buffer_322_out, controlled_buffer_323_out, controlled_buffer_324_out,
       controlled_buffer_325_out, controlled_buffer_326_out, controlled_buffer_327_out,
       controlled_buffer_328_out, controlled_buffer_329_out, controlled_buffer_330_out,
       controlled_buffer_332_out, controlled_buffer_334_out, controlled_buffer_336_out,
       controlled_buffer_338_out, controlled_buffer_340_out, controlled_buffer_342_out,
       controlled_buffer_343_out, controlled_buffer_344_out, controlled_buffer_345_out,
       controlled_buffer_353_out, controlled_buffer_354_out, controlled_buffer_355_out,
       controlled_buffer_356_out, controlled_buffer_357_out, controlled_buffer_358_out,
       controlled_buffer_359_out, controlled_buffer_360_out, controlled_buffer_361_out,
       controlled_buffer_369_out, controlled_buffer_370_out, controlled_buffer_371_out,
       controlled_buffer_372_out, controlled_buffer_373_out, controlled_buffer_374_out,
       controlled_buffer_375_out, controlled_buffer_376_out, controlled_buffer_377_out, d_ff_1_qn, d_ff_2_qn,
       d_ff_3_qn, d_ff_4_qn, d_ff_5_qn, d_ff_6_qn, d_ff_7_qn, d_ff_8_qn, d_ff_9_qn, d_ff_10_qn, d_ff_11_qn,
       d_ff_12_qn, d_ff_13_qn, d_ff_14_qn, d_ff_15_qn, d_ff_16_qn, d_ff_17_qn, d_ff_18_qn, d_ff_19_qn,
       d_ff_20_qn, d_ff_21_qn, d_ff_22_qn, d_ff_23_qn, d_ff_24_qn, d_ff_25_qn, d_ff_26_qn, d_ff_27_qn,
       d_ff_28_qn, d_ff_29_qn, d_ff_30_qn, d_ff_31_qn, d_ff_32_qn, d_ff_33_qn, d_ff_34_qn, d_ff_35_qn,
       d_ff_36_qn, d_ff_37_qn, d_ff_38_qn, d_ff_39_qn, d_ff_40_qn, d_ff_41_qn, d_ff_42_qn, d_ff_43_qn,
       d_ff_44_qn, d_ff_45_qn, d_ff_46_qn, d_ff_47_qn, d_ff_48_qn, d_ff_49_qn, d_ff_50_qn, d_ff_51_qn,
       d_ff_52_qn, d_ff_53_qn, d_ff_54_qn, d_ff_55_qn, d_ff_56_qn, d_ff_57_qn, d_ff_58_qn, d_ff_59_qn,
       d_ff_60_qn, d_ff_61_qn, d_ff_62_qn, d_ff_63_qn, d_ff_64_qn, d_ff_65_qn, d_ff_66_qn, d_ff_67_qn,
       d_ff_68_qn, d_ff_69_qn, d_ff_70_qn, d_ff_71_qn, d_ff_72_qn, d_ff_73_qn, d_ff_74_qn, d_ff_75_qn,
       d_ff_76_qn, d_ff_77_qn, d_ff_78_qn, d_ff_79_qn, d_ff_80_qn, d_ff_81_qn, d_ff_82_qn, d_ff_83_qn,
       d_ff_84_qn, d_ff_85_qn, d_ff_86_qn, d_ff_87_qn, d_ff_88_qn, d_ff_89_qn, d_ff_90_qn, d_ff_91_qn,
       d_ff_92_qn, d_ff_93_qn, d_ff_94_qn, d_ff_95_qn, d_ff_96_qn, d_ff_97_qn, d_ff_98_qn, d_ff_99_qn,
       d_ff_100_qn, d_ff_101_qn, d_ff_102_qn, d_ff_103_qn, d_ff_104_qn, d_ff_105_qn, d_ff_106_qn,
       d_ff_107_qn, d_ff_108_qn, d_ff_109_qn, d_ff_110_qn, d_ff_111_qn, d_ff_112_qn, d_ff_113_qn,
       d_ff_114_qn, d_ff_115_qn, d_ff_116_qn, d_ff_117_qn, d_ff_118_qn, d_ff_119_qn, d_ff_120_qn,
       d_ff_121_qn, d_ff_122_qn, d_ff_123_qn, d_ff_124_qn, d_ff_125_qn, d_ff_126_qn, d_ff_127_qn,
       d_ff_128_qn, d_ff_129_qn, d_ff_130_qn, d_ff_131_qn, d_ff_132_qn, d_ff_133_qn, d_ff_134_qn,
       d_ff_135_qn, d_ff_136_qn, d_ff_137_qn, d_ff_138_qn, d_ff_139_qn, d_ff_140_qn, d_ff_141_qn,
       d_ff_142_qn, d_ff_143_qn, d_ff_144_qn, d_ff_145_qn, d_ff_146_qn, d_ff_147_qn, d_ff_148_qn,
       d_ff_149_qn, d_ff_150_qn, d_ff_151_qn, d_ff_152_qn, d_ff_153_qn, d_ff_154_qn, d_ff_155_qn,
       d_ff_156_qn, d_ff_157_qn, d_ff_158_qn, d_ff_159_qn, d_ff_160_qn, d_ff_161_qn, d_ff_162_qn,
       d_ff_163_qn, d_ff_164_qn, d_ff_165_qn, d_ff_166_qn, d_ff_167_qn, d_ff_168_qn, multiplexer_1_out,
       multiplexer_3_out, multiplexer_5_out, multiplexer_7_out, multiplexer_9_out, multiplexer_11_out,
       nor_1_out, nor_2_out, nor_3_out, nor_4_out, nor_5_out, nor_6_out, nor_7_out, nor_8_out, nor_9_out,
       nor_10_out, nor_11_out, not_1_out, not_2_out, not_3_out, not_4_out, not_5_out, not_6_out;

  not not_1 (not_1_out, PAL4);
  not not_2 (not_2_out, PAL0);
  not not_3 (not_3_out, PAL1);
  not not_4 (not_4_out, PAL2);
  not not_5 (not_5_out, PAL3);
  nor nor_1 (nor_1_out, PAL0, PAL1);
  nor nor_2 (nor_2_out, not_4_out, not_5_out);
  nor nor_3 (nor_3_out, not_1_out, PAL0, not_3_out);
  nor nor_4 (nor_4_out, PAL2, not_5_out);
  nor nor_5 (nor_5_out, PAL4, PAL0, not_3_out);
  nor nor_6 (nor_6_out, not_4_out, PAL3);
  nor nor_7 (nor_7_out, not_1_out, not_2_out, PAL1);
  nor nor_8 (nor_8_out, PAL2, PAL3);
  nor nor_9 (nor_9_out, PAL4, not_2_out, PAL1);
  nor nor_10 (nor_10_out, not_1_out, not_2_out, not_3_out);
  nor nor_11 (nor_11_out, PAL4, not_2_out, not_3_out);
  not not_6 (not_6_out, PCLK);
  and and_1 (and_1_out, nor_1_out, not_6_out);
  and and_2 (and_2_out, nor_3_out, not_6_out);
  and and_3 (and_3_out, nor_5_out, not_6_out);
  and and_4 (and_4_out, nor_7_out, not_6_out);
  and and_5 (and_5_out, nor_9_out, not_6_out);
  and and_6 (and_6_out, nor_10_out, not_6_out);
  and and_7 (and_7_out, nor_11_out, not_6_out);
  assign controlled_buffer_1_out = and_1_out ? controlled_buffer_8_out : 1'bz;  // Controlled_Buffer controlled_buffer_1
  assign controlled_buffer_2_out = and_2_out ? controlled_buffer_8_out : 1'bz;  // Controlled_Buffer controlled_buffer_2
  assign controlled_buffer_3_out = and_3_out ? controlled_buffer_8_out : 1'bz;  // Controlled_Buffer controlled_buffer_3
  assign controlled_buffer_4_out = and_4_out ? controlled_buffer_8_out : 1'bz;  // Controlled_Buffer controlled_buffer_4
  assign controlled_buffer_5_out = and_5_out ? controlled_buffer_8_out : 1'bz;  // Controlled_Buffer controlled_buffer_5
  assign controlled_buffer_6_out = and_6_out ? controlled_buffer_8_out : 1'bz;  // Controlled_Buffer controlled_buffer_6
  assign controlled_buffer_7_out = and_7_out ? controlled_buffer_8_out : 1'bz;  // Controlled_Buffer controlled_buffer_7
  assign controlled_buffer_8_out = nor_2_out ? multiplexer_1_out : 1'bz;  // Controlled_Buffer controlled_buffer_8
  assign controlled_buffer_9_out = and_1_out ? d_ff_1_qn : 1'bz;  // Controlled_Buffer controlled_buffer_9
  D_Flip_Flop #(.trigger("high")) d_ff_1 (
    .clk(1'b1), .D(controlled_buffer_1_out), .Qn(d_ff_1_qn));  // open: Q, preset, en, reset
  D_Flip_Flop #(.trigger("high")) d_ff_2 (
    .clk(1'b1), .D(controlled_buffer_2_out), .Qn(d_ff_2_qn));  // open: Q, preset, en, reset
  assign controlled_buffer_9_out = and_2_out ? d_ff_2_qn : 1'bz;  // Controlled_Buffer controlled_buffer_10
  assign controlled_buffer_9_out = and_3_out ? d_ff_3_qn : 1'bz;  // Controlled_Buffer controlled_buffer_11
  D_Flip_Flop #(.trigger("high")) d_ff_3 (
    .clk(1'b1), .D(controlled_buffer_3_out), .Qn(d_ff_3_qn));  // open: Q, preset, en, reset
  assign controlled_buffer_9_out = and_4_out ? d_ff_4_qn : 1'bz;  // Controlled_Buffer controlled_buffer_12
  D_Flip_Flop #(.trigger("high")) d_ff_4 (
    .clk(1'b1), .D(controlled_buffer_4_out), .Qn(d_ff_4_qn));  // open: Q, preset, en, reset
  D_Flip_Flop #(.trigger("high")) d_ff_5 (
    .clk(1'b1), .D(controlled_buffer_5_out), .Qn(d_ff_5_qn));  // open: Q, preset, en, reset
  assign controlled_buffer_9_out = and_5_out ? d_ff_5_qn : 1'bz;  // Controlled_Buffer controlled_buffer_13
  assign controlled_buffer_9_out = and_6_out ? d_ff_6_qn : 1'bz;  // Controlled_Buffer controlled_buffer_14
  D_Flip_Flop #(.trigger("high")) d_ff_6 (
    .clk(1'b1), .D(controlled_buffer_6_out), .Qn(d_ff_6_qn));  // open: Q, preset, en, reset
  D_Flip_Flop #(.trigger("high")) d_ff_7 (
    .clk(1'b1), .D(controlled_buffer_7_out), .Qn(d_ff_7_qn));  // open: Q, preset, en, reset
  assign controlled_buffer_9_out = and_7_out ? d_ff_7_qn : 1'bz;  // Controlled_Buffer controlled_buffer_15
  assign controlled_buffer_16_out = nor_2_out ? controlled_buffer_9_out : 1'bz;  // Controlled_Buffer controlled_buffer_16
  Multiplexer #(.enable("false")) multiplexer_1 (.in0(CB3_RAM), .in1(1'b1), .out(multiplexer_1_out), .sel(PCLK));
  assign controlled_buffer_17_out = and_1_out ? controlled_buffer_24_out : 1'bz;  // Controlled_Buffer controlled_buffer_17
  assign controlled_buffer_18_out = and_2_out ? controlled_buffer_24_out : 1'bz;  // Controlled_Buffer controlled_buffer_18
  assign controlled_buffer_19_out = and_3_out ? controlled_buffer_24_out : 1'bz;  // Controlled_Buffer controlled_buffer_19
  assign controlled_buffer_20_out = and_4_out ? controlled_buffer_24_out : 1'bz;  // Controlled_Buffer controlled_buffer_20
  assign controlled_buffer_21_out = and_5_out ? controlled_buffer_24_out : 1'bz;  // Controlled_Buffer controlled_buffer_21
  assign controlled_buffer_22_out = and_6_out ? controlled_buffer_24_out : 1'bz;  // Controlled_Buffer controlled_buffer_22
  assign controlled_buffer_23_out = and_7_out ? controlled_buffer_24_out : 1'bz;  // Controlled_Buffer controlled_buffer_23
  assign controlled_buffer_24_out = nor_4_out ? multiplexer_1_out : 1'bz;  // Controlled_Buffer controlled_buffer_24
  D_Flip_Flop #(.trigger("high")) d_ff_8 (
    .clk(1'b1), .D(controlled_buffer_17_out), .Qn(d_ff_8_qn));  // open: Q, preset, en, reset
  assign controlled_buffer_25_out = and_1_out ? d_ff_8_qn : 1'bz;  // Controlled_Buffer controlled_buffer_25
  assign controlled_buffer_25_out = and_2_out ? d_ff_9_qn : 1'bz;  // Controlled_Buffer controlled_buffer_26
  D_Flip_Flop #(.trigger("high")) d_ff_9 (
    .clk(1'b1), .D(controlled_buffer_18_out), .Qn(d_ff_9_qn));  // open: Q, preset, en, reset
  D_Flip_Flop #(.trigger("high")) d_ff_10 (
    .clk(1'b1), .D(controlled_buffer_19_out), .Qn(d_ff_10_qn));  // open: Q, preset, en, reset
  assign controlled_buffer_25_out = and_3_out ? d_ff_10_qn : 1'bz;  // Controlled_Buffer controlled_buffer_27
  D_Flip_Flop #(.trigger("high")) d_ff_11 (
    .clk(1'b1), .D(controlled_buffer_20_out), .Qn(d_ff_11_qn));  // open: Q, preset, en, reset
  assign controlled_buffer_25_out = and_4_out ? d_ff_11_qn : 1'bz;  // Controlled_Buffer controlled_buffer_28
  assign controlled_buffer_25_out = and_5_out ? d_ff_12_qn : 1'bz;  // Controlled_Buffer controlled_buffer_29
  D_Flip_Flop #(.trigger("high")) d_ff_12 (
    .clk(1'b1), .D(controlled_buffer_21_out), .Qn(d_ff_12_qn));  // open: Q, preset, en, reset
  D_Flip_Flop #(.trigger("high")) d_ff_13 (
    .clk(1'b1), .D(controlled_buffer_22_out), .Qn(d_ff_13_qn));  // open: Q, preset, en, reset
  assign controlled_buffer_25_out = and_6_out ? d_ff_13_qn : 1'bz;  // Controlled_Buffer controlled_buffer_30
  assign controlled_buffer_25_out = and_7_out ? d_ff_14_qn : 1'bz;  // Controlled_Buffer controlled_buffer_31
  D_Flip_Flop #(.trigger("high")) d_ff_14 (
    .clk(1'b1), .D(controlled_buffer_23_out), .Qn(d_ff_14_qn));  // open: Q, preset, en, reset
  assign controlled_buffer_32_out = nor_6_out ? multiplexer_1_out : 1'bz;  // Controlled_Buffer controlled_buffer_32
  assign controlled_buffer_16_out = nor_4_out ? controlled_buffer_25_out : 1'bz;  // Controlled_Buffer controlled_buffer_33
  D_Flip_Flop #(.trigger("high")) d_ff_15 (
    .clk(1'b1), .D(controlled_buffer_34_out), .Qn(d_ff_15_qn));  // open: Q, preset, en, reset
  assign controlled_buffer_34_out = and_1_out ? controlled_buffer_32_out : 1'bz;  // Controlled_Buffer controlled_buffer_34
  D_Flip_Flop #(.trigger("high")) d_ff_16 (
    .clk(1'b1), .D(controlled_buffer_35_out), .Qn(d_ff_16_qn));  // open: Q, preset, en, reset
  assign controlled_buffer_35_out = and_2_out ? controlled_buffer_32_out : 1'bz;  // Controlled_Buffer controlled_buffer_35
  D_Flip_Flop #(.trigger("high")) d_ff_17 (
    .clk(1'b1), .D(controlled_buffer_36_out), .Qn(d_ff_17_qn));  // open: Q, preset, en, reset
  assign controlled_buffer_36_out = and_3_out ? controlled_buffer_32_out : 1'bz;  // Controlled_Buffer controlled_buffer_36
  D_Flip_Flop #(.trigger("high")) d_ff_18 (
    .clk(1'b1), .D(controlled_buffer_37_out), .Qn(d_ff_18_qn));  // open: Q, preset, en, reset
  assign controlled_buffer_37_out = and_4_out ? controlled_buffer_32_out : 1'bz;  // Controlled_Buffer controlled_buffer_37
  D_Flip_Flop #(.trigger("high")) d_ff_19 (
    .clk(1'b1), .D(controlled_buffer_38_out), .Qn(d_ff_19_qn));  // open: Q, preset, en, reset
  assign controlled_buffer_38_out = and_5_out ? controlled_buffer_32_out : 1'bz;  // Controlled_Buffer controlled_buffer_38
  D_Flip_Flop #(.trigger("high")) d_ff_20 (
    .clk(1'b1), .D(controlled_buffer_39_out), .Qn(d_ff_20_qn));  // open: Q, preset, en, reset
  assign controlled_buffer_39_out = and_6_out ? controlled_buffer_32_out : 1'bz;  // Controlled_Buffer controlled_buffer_39
  D_Flip_Flop #(.trigger("high")) d_ff_21 (
    .clk(1'b1), .D(controlled_buffer_40_out), .Qn(d_ff_21_qn));  // open: Q, preset, en, reset
  assign controlled_buffer_40_out = and_7_out ? controlled_buffer_32_out : 1'bz;  // Controlled_Buffer controlled_buffer_40
  assign controlled_buffer_41_out = and_1_out ? d_ff_15_qn : 1'bz;  // Controlled_Buffer controlled_buffer_41
  assign controlled_buffer_42_out = and_1_out ? controlled_buffer_56_out : 1'bz;  // Controlled_Buffer controlled_buffer_42
  assign controlled_buffer_41_out = and_2_out ? d_ff_16_qn : 1'bz;  // Controlled_Buffer controlled_buffer_43
  assign controlled_buffer_44_out = and_2_out ? controlled_buffer_56_out : 1'bz;  // Controlled_Buffer controlled_buffer_44
  assign controlled_buffer_41_out = and_3_out ? d_ff_17_qn : 1'bz;  // Controlled_Buffer controlled_buffer_45
  assign controlled_buffer_46_out = and_3_out ? controlled_buffer_56_out : 1'bz;  // Controlled_Buffer controlled_buffer_46
  assign controlled_buffer_41_out = and_4_out ? d_ff_18_qn : 1'bz;  // Controlled_Buffer controlled_buffer_47
  assign controlled_buffer_48_out = and_4_out ? controlled_buffer_56_out : 1'bz;  // Controlled_Buffer controlled_buffer_48
  assign controlled_buffer_41_out = and_5_out ? d_ff_19_qn : 1'bz;  // Controlled_Buffer controlled_buffer_49
  assign controlled_buffer_50_out = and_5_out ? controlled_buffer_56_out : 1'bz;  // Controlled_Buffer controlled_buffer_50
  assign controlled_buffer_41_out = and_6_out ? d_ff_20_qn : 1'bz;  // Controlled_Buffer controlled_buffer_51
  assign controlled_buffer_52_out = and_6_out ? controlled_buffer_56_out : 1'bz;  // Controlled_Buffer controlled_buffer_52
  assign controlled_buffer_41_out = and_7_out ? d_ff_21_qn : 1'bz;  // Controlled_Buffer controlled_buffer_53
  assign controlled_buffer_54_out = and_7_out ? controlled_buffer_56_out : 1'bz;  // Controlled_Buffer controlled_buffer_54
  assign controlled_buffer_16_out = nor_6_out ? controlled_buffer_41_out : 1'bz;  // Controlled_Buffer controlled_buffer_55
  assign controlled_buffer_56_out = nor_8_out ? multiplexer_1_out : 1'bz;  // Controlled_Buffer controlled_buffer_56
  assign controlled_buffer_57_out = and_1_out ? d_ff_22_qn : 1'bz;  // Controlled_Buffer controlled_buffer_57
  D_Flip_Flop #(.trigger("high")) d_ff_22 (
    .clk(1'b1), .D(controlled_buffer_42_out), .Qn(d_ff_22_qn));  // open: Q, preset, en, reset
  assign controlled_buffer_57_out = and_2_out ? d_ff_23_qn : 1'bz;  // Controlled_Buffer controlled_buffer_58
  D_Flip_Flop #(.trigger("high")) d_ff_23 (
    .clk(1'b1), .D(controlled_buffer_44_out), .Qn(d_ff_23_qn));  // open: Q, preset, en, reset
  assign controlled_buffer_57_out = and_3_out ? d_ff_24_qn : 1'bz;  // Controlled_Buffer controlled_buffer_59
  D_Flip_Flop #(.trigger("high")) d_ff_24 (
    .clk(1'b1), .D(controlled_buffer_46_out), .Qn(d_ff_24_qn));  // open: Q, preset, en, reset
  D_Flip_Flop #(.trigger("high")) d_ff_25 (
    .clk(1'b1), .D(controlled_buffer_48_out), .Qn(d_ff_25_qn));  // open: Q, preset, en, reset
  assign controlled_buffer_57_out = and_4_out ? d_ff_25_qn : 1'bz;  // Controlled_Buffer controlled_buffer_60
  D_Flip_Flop #(.trigger("high")) d_ff_26 (
    .clk(1'b1), .D(controlled_buffer_50_out), .Qn(d_ff_26_qn));  // open: Q, preset, en, reset
  assign controlled_buffer_57_out = and_5_out ? d_ff_26_qn : 1'bz;  // Controlled_Buffer controlled_buffer_61
  D_Flip_Flop #(.trigger("high")) d_ff_27 (
    .clk(1'b1), .D(controlled_buffer_52_out), .Qn(d_ff_27_qn));  // open: Q, preset, en, reset
  assign controlled_buffer_57_out = and_6_out ? d_ff_27_qn : 1'bz;  // Controlled_Buffer controlled_buffer_62
  D_Flip_Flop #(.trigger("high")) d_ff_28 (
    .clk(1'b1), .D(controlled_buffer_54_out), .Qn(d_ff_28_qn));  // open: Q, preset, en, reset
  assign controlled_buffer_57_out = and_7_out ? d_ff_28_qn : 1'bz;  // Controlled_Buffer controlled_buffer_63
  assign controlled_buffer_16_out = nor_8_out ? controlled_buffer_57_out : 1'bz;  // Controlled_Buffer controlled_buffer_64
  Multiplexer #(.enable("false")) multiplexer_2 (.in0(controlled_buffer_16_out), .in1(1'b1), .out(RAM_CB3), .sel(PCLK));
  assign controlled_buffer_65_out = and_1_out ? controlled_buffer_72_out : 1'bz;  // Controlled_Buffer controlled_buffer_65
  assign controlled_buffer_66_out = and_2_out ? controlled_buffer_72_out : 1'bz;  // Controlled_Buffer controlled_buffer_66
  assign controlled_buffer_67_out = and_3_out ? controlled_buffer_72_out : 1'bz;  // Controlled_Buffer controlled_buffer_67
  assign controlled_buffer_68_out = and_4_out ? controlled_buffer_72_out : 1'bz;  // Controlled_Buffer controlled_buffer_68
  assign controlled_buffer_69_out = and_5_out ? controlled_buffer_72_out : 1'bz;  // Controlled_Buffer controlled_buffer_69
  assign controlled_buffer_70_out = and_6_out ? controlled_buffer_72_out : 1'bz;  // Controlled_Buffer controlled_buffer_70
  assign controlled_buffer_71_out = and_7_out ? controlled_buffer_72_out : 1'bz;  // Controlled_Buffer controlled_buffer_71
  assign controlled_buffer_72_out = nor_2_out ? multiplexer_3_out : 1'bz;  // Controlled_Buffer controlled_buffer_72
  D_Flip_Flop #(.trigger("high")) d_ff_29 (
    .clk(1'b1), .D(controlled_buffer_65_out), .Qn(d_ff_29_qn));  // open: Q, preset, en, reset
  assign controlled_buffer_73_out = and_1_out ? d_ff_29_qn : 1'bz;  // Controlled_Buffer controlled_buffer_73
  assign controlled_buffer_73_out = and_2_out ? d_ff_30_qn : 1'bz;  // Controlled_Buffer controlled_buffer_74
  D_Flip_Flop #(.trigger("high")) d_ff_30 (
    .clk(1'b1), .D(controlled_buffer_66_out), .Qn(d_ff_30_qn));  // open: Q, preset, en, reset
  D_Flip_Flop #(.trigger("high")) d_ff_31 (
    .clk(1'b1), .D(controlled_buffer_67_out), .Qn(d_ff_31_qn));  // open: Q, preset, en, reset
  assign controlled_buffer_73_out = and_3_out ? d_ff_31_qn : 1'bz;  // Controlled_Buffer controlled_buffer_75
  assign controlled_buffer_73_out = and_4_out ? d_ff_32_qn : 1'bz;  // Controlled_Buffer controlled_buffer_76
  D_Flip_Flop #(.trigger("high")) d_ff_32 (
    .clk(1'b1), .D(controlled_buffer_68_out), .Qn(d_ff_32_qn));  // open: Q, preset, en, reset
  assign controlled_buffer_73_out = and_5_out ? d_ff_33_qn : 1'bz;  // Controlled_Buffer controlled_buffer_77
  D_Flip_Flop #(.trigger("high")) d_ff_33 (
    .clk(1'b1), .D(controlled_buffer_69_out), .Qn(d_ff_33_qn));  // open: Q, preset, en, reset
  D_Flip_Flop #(.trigger("high")) d_ff_34 (
    .clk(1'b1), .D(controlled_buffer_70_out), .Qn(d_ff_34_qn));  // open: Q, preset, en, reset
  assign controlled_buffer_73_out = and_6_out ? d_ff_34_qn : 1'bz;  // Controlled_Buffer controlled_buffer_78
  assign controlled_buffer_73_out = and_7_out ? d_ff_35_qn : 1'bz;  // Controlled_Buffer controlled_buffer_79
  D_Flip_Flop #(.trigger("high")) d_ff_35 (
    .clk(1'b1), .D(controlled_buffer_71_out), .Qn(d_ff_35_qn));  // open: Q, preset, en, reset
  assign controlled_buffer_80_out = nor_2_out ? controlled_buffer_73_out : 1'bz;  // Controlled_Buffer controlled_buffer_80
  Multiplexer #(.enable("false")) multiplexer_3 (.in0(CB2_RAM), .in1(1'b1), .out(multiplexer_3_out), .sel(PCLK));
  assign controlled_buffer_81_out = and_1_out ? controlled_buffer_88_out : 1'bz;  // Controlled_Buffer controlled_buffer_81
  assign controlled_buffer_82_out = and_2_out ? controlled_buffer_88_out : 1'bz;  // Controlled_Buffer controlled_buffer_82
  assign controlled_buffer_83_out = and_3_out ? controlled_buffer_88_out : 1'bz;  // Controlled_Buffer controlled_buffer_83
  assign controlled_buffer_84_out = and_4_out ? controlled_buffer_88_out : 1'bz;  // Controlled_Buffer controlled_buffer_84
  assign controlled_buffer_85_out = and_5_out ? controlled_buffer_88_out : 1'bz;  // Controlled_Buffer controlled_buffer_85
  assign controlled_buffer_86_out = and_6_out ? controlled_buffer_88_out : 1'bz;  // Controlled_Buffer controlled_buffer_86
  assign controlled_buffer_87_out = and_7_out ? controlled_buffer_88_out : 1'bz;  // Controlled_Buffer controlled_buffer_87
  assign controlled_buffer_88_out = nor_4_out ? multiplexer_3_out : 1'bz;  // Controlled_Buffer controlled_buffer_88
  D_Flip_Flop #(.trigger("high")) d_ff_36 (
    .clk(1'b1), .D(controlled_buffer_81_out), .Qn(d_ff_36_qn));  // open: Q, preset, en, reset
  assign controlled_buffer_89_out = and_1_out ? d_ff_36_qn : 1'bz;  // Controlled_Buffer controlled_buffer_89
  D_Flip_Flop #(.trigger("high")) d_ff_37 (
    .clk(1'b1), .D(controlled_buffer_82_out), .Qn(d_ff_37_qn));  // open: Q, preset, en, reset
  assign controlled_buffer_89_out = and_2_out ? d_ff_37_qn : 1'bz;  // Controlled_Buffer controlled_buffer_90
  D_Flip_Flop #(.trigger("high")) d_ff_38 (
    .clk(1'b1), .D(controlled_buffer_83_out), .Qn(d_ff_38_qn));  // open: Q, preset, en, reset
  assign controlled_buffer_89_out = and_3_out ? d_ff_38_qn : 1'bz;  // Controlled_Buffer controlled_buffer_91
  D_Flip_Flop #(.trigger("high")) d_ff_39 (
    .clk(1'b1), .D(controlled_buffer_84_out), .Qn(d_ff_39_qn));  // open: Q, preset, en, reset
  assign controlled_buffer_89_out = and_4_out ? d_ff_39_qn : 1'bz;  // Controlled_Buffer controlled_buffer_92
  D_Flip_Flop #(.trigger("high")) d_ff_40 (
    .clk(1'b1), .D(controlled_buffer_85_out), .Qn(d_ff_40_qn));  // open: Q, preset, en, reset
  assign controlled_buffer_89_out = and_5_out ? d_ff_40_qn : 1'bz;  // Controlled_Buffer controlled_buffer_93
  assign controlled_buffer_89_out = and_6_out ? d_ff_41_qn : 1'bz;  // Controlled_Buffer controlled_buffer_94
  D_Flip_Flop #(.trigger("high")) d_ff_41 (
    .clk(1'b1), .D(controlled_buffer_86_out), .Qn(d_ff_41_qn));  // open: Q, preset, en, reset
  D_Flip_Flop #(.trigger("high")) d_ff_42 (
    .clk(1'b1), .D(controlled_buffer_87_out), .Qn(d_ff_42_qn));  // open: Q, preset, en, reset
  assign controlled_buffer_89_out = and_7_out ? d_ff_42_qn : 1'bz;  // Controlled_Buffer controlled_buffer_95
  assign controlled_buffer_96_out = nor_6_out ? multiplexer_3_out : 1'bz;  // Controlled_Buffer controlled_buffer_96
  assign controlled_buffer_80_out = nor_4_out ? controlled_buffer_89_out : 1'bz;  // Controlled_Buffer controlled_buffer_97
  D_Flip_Flop #(.trigger("high")) d_ff_43 (
    .clk(1'b1), .D(controlled_buffer_98_out), .Qn(d_ff_43_qn));  // open: Q, preset, en, reset
  assign controlled_buffer_98_out = and_1_out ? controlled_buffer_96_out : 1'bz;  // Controlled_Buffer controlled_buffer_98
  D_Flip_Flop #(.trigger("high")) d_ff_44 (
    .clk(1'b1), .D(controlled_buffer_99_out), .Qn(d_ff_44_qn));  // open: Q, preset, en, reset
  assign controlled_buffer_99_out = and_2_out ? controlled_buffer_96_out : 1'bz;  // Controlled_Buffer controlled_buffer_99
  D_Flip_Flop #(.trigger("high")) d_ff_45 (
    .clk(1'b1), .D(controlled_buffer_100_out), .Qn(d_ff_45_qn));  // open: Q, preset, en, reset
  assign controlled_buffer_100_out = and_3_out ? controlled_buffer_96_out : 1'bz;  // Controlled_Buffer controlled_buffer_100
  D_Flip_Flop #(.trigger("high")) d_ff_46 (
    .clk(1'b1), .D(controlled_buffer_101_out), .Qn(d_ff_46_qn));  // open: Q, preset, en, reset
  assign controlled_buffer_101_out = and_4_out ? controlled_buffer_96_out : 1'bz;  // Controlled_Buffer controlled_buffer_101
  D_Flip_Flop #(.trigger("high")) d_ff_47 (
    .clk(1'b1), .D(controlled_buffer_102_out), .Qn(d_ff_47_qn));  // open: Q, preset, en, reset
  assign controlled_buffer_102_out = and_5_out ? controlled_buffer_96_out : 1'bz;  // Controlled_Buffer controlled_buffer_102
  D_Flip_Flop #(.trigger("high")) d_ff_48 (
    .clk(1'b1), .D(controlled_buffer_103_out), .Qn(d_ff_48_qn));  // open: Q, preset, en, reset
  assign controlled_buffer_103_out = and_6_out ? controlled_buffer_96_out : 1'bz;  // Controlled_Buffer controlled_buffer_103
  D_Flip_Flop #(.trigger("high")) d_ff_49 (
    .clk(1'b1), .D(controlled_buffer_104_out), .Qn(d_ff_49_qn));  // open: Q, preset, en, reset
  assign controlled_buffer_104_out = and_7_out ? controlled_buffer_96_out : 1'bz;  // Controlled_Buffer controlled_buffer_104
  assign controlled_buffer_105_out = and_1_out ? d_ff_43_qn : 1'bz;  // Controlled_Buffer controlled_buffer_105
  assign controlled_buffer_106_out = and_1_out ? controlled_buffer_120_out : 1'bz;  // Controlled_Buffer controlled_buffer_106
  assign controlled_buffer_105_out = and_2_out ? d_ff_44_qn : 1'bz;  // Controlled_Buffer controlled_buffer_107
  assign controlled_buffer_108_out = and_2_out ? controlled_buffer_120_out : 1'bz;  // Controlled_Buffer controlled_buffer_108
  assign controlled_buffer_105_out = and_3_out ? d_ff_45_qn : 1'bz;  // Controlled_Buffer controlled_buffer_109
  assign controlled_buffer_110_out = and_3_out ? controlled_buffer_120_out : 1'bz;  // Controlled_Buffer controlled_buffer_110
  assign controlled_buffer_105_out = and_4_out ? d_ff_46_qn : 1'bz;  // Controlled_Buffer controlled_buffer_111
  assign controlled_buffer_112_out = and_4_out ? controlled_buffer_120_out : 1'bz;  // Controlled_Buffer controlled_buffer_112
  assign controlled_buffer_105_out = and_5_out ? d_ff_47_qn : 1'bz;  // Controlled_Buffer controlled_buffer_113
  assign controlled_buffer_114_out = and_5_out ? controlled_buffer_120_out : 1'bz;  // Controlled_Buffer controlled_buffer_114
  assign controlled_buffer_105_out = and_6_out ? d_ff_48_qn : 1'bz;  // Controlled_Buffer controlled_buffer_115
  assign controlled_buffer_116_out = and_6_out ? controlled_buffer_120_out : 1'bz;  // Controlled_Buffer controlled_buffer_116
  assign controlled_buffer_105_out = and_7_out ? d_ff_49_qn : 1'bz;  // Controlled_Buffer controlled_buffer_117
  assign controlled_buffer_118_out = and_7_out ? controlled_buffer_120_out : 1'bz;  // Controlled_Buffer controlled_buffer_118
  assign controlled_buffer_80_out = nor_6_out ? controlled_buffer_105_out : 1'bz;  // Controlled_Buffer controlled_buffer_119
  assign controlled_buffer_120_out = nor_8_out ? multiplexer_3_out : 1'bz;  // Controlled_Buffer controlled_buffer_120
  assign controlled_buffer_121_out = and_1_out ? d_ff_50_qn : 1'bz;  // Controlled_Buffer controlled_buffer_121
  D_Flip_Flop #(.trigger("high")) d_ff_50 (
    .clk(1'b1), .D(controlled_buffer_106_out), .Qn(d_ff_50_qn));  // open: Q, preset, en, reset
  assign controlled_buffer_121_out = and_2_out ? d_ff_51_qn : 1'bz;  // Controlled_Buffer controlled_buffer_122
  D_Flip_Flop #(.trigger("high")) d_ff_51 (
    .clk(1'b1), .D(controlled_buffer_108_out), .Qn(d_ff_51_qn));  // open: Q, preset, en, reset
  D_Flip_Flop #(.trigger("high")) d_ff_52 (
    .clk(1'b1), .D(controlled_buffer_110_out), .Qn(d_ff_52_qn));  // open: Q, preset, en, reset
  assign controlled_buffer_121_out = and_3_out ? d_ff_52_qn : 1'bz;  // Controlled_Buffer controlled_buffer_123
  D_Flip_Flop #(.trigger("high")) d_ff_53 (
    .clk(1'b1), .D(controlled_buffer_112_out), .Qn(d_ff_53_qn));  // open: Q, preset, en, reset
  assign controlled_buffer_121_out = and_4_out ? d_ff_53_qn : 1'bz;  // Controlled_Buffer controlled_buffer_124
  assign controlled_buffer_121_out = and_5_out ? d_ff_54_qn : 1'bz;  // Controlled_Buffer controlled_buffer_125
  D_Flip_Flop #(.trigger("high")) d_ff_54 (
    .clk(1'b1), .D(controlled_buffer_114_out), .Qn(d_ff_54_qn));  // open: Q, preset, en, reset
  D_Flip_Flop #(.trigger("high")) d_ff_55 (
    .clk(1'b1), .D(controlled_buffer_116_out), .Qn(d_ff_55_qn));  // open: Q, preset, en, reset
  assign controlled_buffer_121_out = and_6_out ? d_ff_55_qn : 1'bz;  // Controlled_Buffer controlled_buffer_126
  D_Flip_Flop #(.trigger("high")) d_ff_56 (
    .clk(1'b1), .D(controlled_buffer_118_out), .Qn(d_ff_56_qn));  // open: Q, preset, en, reset
  assign controlled_buffer_121_out = and_7_out ? d_ff_56_qn : 1'bz;  // Controlled_Buffer controlled_buffer_127
  assign controlled_buffer_80_out = nor_8_out ? controlled_buffer_121_out : 1'bz;  // Controlled_Buffer controlled_buffer_128
  Multiplexer #(.enable("false")) multiplexer_4 (.in0(controlled_buffer_80_out), .in1(1'b1), .out(RAM_CB2), .sel(PCLK));
  assign controlled_buffer_129_out = and_1_out ? controlled_buffer_136_out : 1'bz;  // Controlled_Buffer controlled_buffer_129
  assign controlled_buffer_130_out = and_2_out ? controlled_buffer_136_out : 1'bz;  // Controlled_Buffer controlled_buffer_130
  assign controlled_buffer_131_out = and_3_out ? controlled_buffer_136_out : 1'bz;  // Controlled_Buffer controlled_buffer_131
  assign controlled_buffer_132_out = and_4_out ? controlled_buffer_136_out : 1'bz;  // Controlled_Buffer controlled_buffer_132
  assign controlled_buffer_133_out = and_5_out ? controlled_buffer_136_out : 1'bz;  // Controlled_Buffer controlled_buffer_133
  assign controlled_buffer_134_out = and_6_out ? controlled_buffer_136_out : 1'bz;  // Controlled_Buffer controlled_buffer_134
  assign controlled_buffer_135_out = and_7_out ? controlled_buffer_136_out : 1'bz;  // Controlled_Buffer controlled_buffer_135
  assign controlled_buffer_136_out = nor_2_out ? multiplexer_5_out : 1'bz;  // Controlled_Buffer controlled_buffer_136
  D_Flip_Flop #(.trigger("high")) d_ff_57 (
    .clk(1'b1), .D(controlled_buffer_129_out), .Qn(d_ff_57_qn));  // open: Q, preset, en, reset
  assign controlled_buffer_137_out = and_1_out ? d_ff_57_qn : 1'bz;  // Controlled_Buffer controlled_buffer_137
  assign controlled_buffer_137_out = and_2_out ? d_ff_58_qn : 1'bz;  // Controlled_Buffer controlled_buffer_138
  D_Flip_Flop #(.trigger("high")) d_ff_58 (
    .clk(1'b1), .D(controlled_buffer_130_out), .Qn(d_ff_58_qn));  // open: Q, preset, en, reset
  assign controlled_buffer_137_out = and_3_out ? d_ff_59_qn : 1'bz;  // Controlled_Buffer controlled_buffer_139
  D_Flip_Flop #(.trigger("high")) d_ff_59 (
    .clk(1'b1), .D(controlled_buffer_131_out), .Qn(d_ff_59_qn));  // open: Q, preset, en, reset
  assign controlled_buffer_137_out = and_4_out ? d_ff_60_qn : 1'bz;  // Controlled_Buffer controlled_buffer_140
  D_Flip_Flop #(.trigger("high")) d_ff_60 (
    .clk(1'b1), .D(controlled_buffer_132_out), .Qn(d_ff_60_qn));  // open: Q, preset, en, reset
  D_Flip_Flop #(.trigger("high")) d_ff_61 (
    .clk(1'b1), .D(controlled_buffer_133_out), .Qn(d_ff_61_qn));  // open: Q, preset, en, reset
  assign controlled_buffer_137_out = and_5_out ? d_ff_61_qn : 1'bz;  // Controlled_Buffer controlled_buffer_141
  D_Flip_Flop #(.trigger("high")) d_ff_62 (
    .clk(1'b1), .D(controlled_buffer_134_out), .Qn(d_ff_62_qn));  // open: Q, preset, en, reset
  assign controlled_buffer_137_out = and_6_out ? d_ff_62_qn : 1'bz;  // Controlled_Buffer controlled_buffer_142
  D_Flip_Flop #(.trigger("high")) d_ff_63 (
    .clk(1'b1), .D(controlled_buffer_135_out), .Qn(d_ff_63_qn));  // open: Q, preset, en, reset
  assign controlled_buffer_137_out = and_7_out ? d_ff_63_qn : 1'bz;  // Controlled_Buffer controlled_buffer_143
  assign controlled_buffer_144_out = nor_4_out ? multiplexer_5_out : 1'bz;  // Controlled_Buffer controlled_buffer_144
  assign controlled_buffer_145_out = nor_2_out ? controlled_buffer_137_out : 1'bz;  // Controlled_Buffer controlled_buffer_145
  Multiplexer #(.enable("false")) multiplexer_5 (.in0(CB1_RAM), .in1(1'b1), .out(multiplexer_5_out), .sel(PCLK));
  assign controlled_buffer_146_out = and_1_out ? controlled_buffer_144_out : 1'bz;  // Controlled_Buffer controlled_buffer_146
  assign controlled_buffer_147_out = and_2_out ? controlled_buffer_144_out : 1'bz;  // Controlled_Buffer controlled_buffer_147
  assign controlled_buffer_148_out = and_3_out ? controlled_buffer_144_out : 1'bz;  // Controlled_Buffer controlled_buffer_148
  assign controlled_buffer_149_out = and_4_out ? controlled_buffer_144_out : 1'bz;  // Controlled_Buffer controlled_buffer_149
  assign controlled_buffer_150_out = and_5_out ? controlled_buffer_144_out : 1'bz;  // Controlled_Buffer controlled_buffer_150
  assign controlled_buffer_151_out = and_6_out ? controlled_buffer_144_out : 1'bz;  // Controlled_Buffer controlled_buffer_151
  assign controlled_buffer_152_out = and_7_out ? controlled_buffer_144_out : 1'bz;  // Controlled_Buffer controlled_buffer_152
  D_Flip_Flop #(.trigger("high")) d_ff_64 (
    .clk(1'b1), .D(controlled_buffer_146_out), .Qn(d_ff_64_qn));  // open: Q, preset, en, reset
  assign controlled_buffer_153_out = and_1_out ? d_ff_64_qn : 1'bz;  // Controlled_Buffer controlled_buffer_153
  D_Flip_Flop #(.trigger("high")) d_ff_65 (
    .clk(1'b1), .D(controlled_buffer_147_out), .Qn(d_ff_65_qn));  // open: Q, preset, en, reset
  assign controlled_buffer_153_out = and_2_out ? d_ff_65_qn : 1'bz;  // Controlled_Buffer controlled_buffer_154
  assign controlled_buffer_153_out = and_3_out ? d_ff_66_qn : 1'bz;  // Controlled_Buffer controlled_buffer_155
  D_Flip_Flop #(.trigger("high")) d_ff_66 (
    .clk(1'b1), .D(controlled_buffer_148_out), .Qn(d_ff_66_qn));  // open: Q, preset, en, reset
  assign controlled_buffer_153_out = and_4_out ? d_ff_67_qn : 1'bz;  // Controlled_Buffer controlled_buffer_156
  D_Flip_Flop #(.trigger("high")) d_ff_67 (
    .clk(1'b1), .D(controlled_buffer_149_out), .Qn(d_ff_67_qn));  // open: Q, preset, en, reset
  D_Flip_Flop #(.trigger("high")) d_ff_68 (
    .clk(1'b1), .D(controlled_buffer_150_out), .Qn(d_ff_68_qn));  // open: Q, preset, en, reset
  assign controlled_buffer_153_out = and_5_out ? d_ff_68_qn : 1'bz;  // Controlled_Buffer controlled_buffer_157
  D_Flip_Flop #(.trigger("high")) d_ff_69 (
    .clk(1'b1), .D(controlled_buffer_151_out), .Qn(d_ff_69_qn));  // open: Q, preset, en, reset
  assign controlled_buffer_153_out = and_6_out ? d_ff_69_qn : 1'bz;  // Controlled_Buffer controlled_buffer_158
  assign controlled_buffer_153_out = and_7_out ? d_ff_70_qn : 1'bz;  // Controlled_Buffer controlled_buffer_159
  D_Flip_Flop #(.trigger("high")) d_ff_70 (
    .clk(1'b1), .D(controlled_buffer_152_out), .Qn(d_ff_70_qn));  // open: Q, preset, en, reset
  assign controlled_buffer_160_out = nor_6_out ? multiplexer_5_out : 1'bz;  // Controlled_Buffer controlled_buffer_160
  assign controlled_buffer_145_out = nor_4_out ? controlled_buffer_153_out : 1'bz;  // Controlled_Buffer controlled_buffer_161
  D_Flip_Flop #(.trigger("high")) d_ff_71 (
    .clk(1'b1), .D(controlled_buffer_162_out), .Qn(d_ff_71_qn));  // open: Q, preset, en, reset
  assign controlled_buffer_162_out = and_1_out ? controlled_buffer_160_out : 1'bz;  // Controlled_Buffer controlled_buffer_162
  D_Flip_Flop #(.trigger("high")) d_ff_72 (
    .clk(1'b1), .D(controlled_buffer_163_out), .Qn(d_ff_72_qn));  // open: Q, preset, en, reset
  assign controlled_buffer_163_out = and_2_out ? controlled_buffer_160_out : 1'bz;  // Controlled_Buffer controlled_buffer_163
  D_Flip_Flop #(.trigger("high")) d_ff_73 (
    .clk(1'b1), .D(controlled_buffer_164_out), .Qn(d_ff_73_qn));  // open: Q, preset, en, reset
  assign controlled_buffer_164_out = and_3_out ? controlled_buffer_160_out : 1'bz;  // Controlled_Buffer controlled_buffer_164
  D_Flip_Flop #(.trigger("high")) d_ff_74 (
    .clk(1'b1), .D(controlled_buffer_165_out), .Qn(d_ff_74_qn));  // open: Q, preset, en, reset
  assign controlled_buffer_165_out = and_4_out ? controlled_buffer_160_out : 1'bz;  // Controlled_Buffer controlled_buffer_165
  D_Flip_Flop #(.trigger("high")) d_ff_75 (
    .clk(1'b1), .D(controlled_buffer_166_out), .Qn(d_ff_75_qn));  // open: Q, preset, en, reset
  assign controlled_buffer_166_out = and_5_out ? controlled_buffer_160_out : 1'bz;  // Controlled_Buffer controlled_buffer_166
  D_Flip_Flop #(.trigger("high")) d_ff_76 (
    .clk(1'b1), .D(controlled_buffer_167_out), .Qn(d_ff_76_qn));  // open: Q, preset, en, reset
  assign controlled_buffer_167_out = and_6_out ? controlled_buffer_160_out : 1'bz;  // Controlled_Buffer controlled_buffer_167
  D_Flip_Flop #(.trigger("high")) d_ff_77 (
    .clk(1'b1), .D(controlled_buffer_168_out), .Qn(d_ff_77_qn));  // open: Q, preset, en, reset
  assign controlled_buffer_168_out = and_7_out ? controlled_buffer_160_out : 1'bz;  // Controlled_Buffer controlled_buffer_168
  assign controlled_buffer_169_out = and_1_out ? d_ff_71_qn : 1'bz;  // Controlled_Buffer controlled_buffer_169
  assign controlled_buffer_170_out = and_1_out ? controlled_buffer_184_out : 1'bz;  // Controlled_Buffer controlled_buffer_170
  assign controlled_buffer_169_out = and_2_out ? d_ff_72_qn : 1'bz;  // Controlled_Buffer controlled_buffer_171
  assign controlled_buffer_172_out = and_2_out ? controlled_buffer_184_out : 1'bz;  // Controlled_Buffer controlled_buffer_172
  assign controlled_buffer_169_out = and_3_out ? d_ff_73_qn : 1'bz;  // Controlled_Buffer controlled_buffer_173
  assign controlled_buffer_174_out = and_3_out ? controlled_buffer_184_out : 1'bz;  // Controlled_Buffer controlled_buffer_174
  assign controlled_buffer_169_out = and_4_out ? d_ff_74_qn : 1'bz;  // Controlled_Buffer controlled_buffer_175
  assign controlled_buffer_176_out = and_4_out ? controlled_buffer_184_out : 1'bz;  // Controlled_Buffer controlled_buffer_176
  assign controlled_buffer_169_out = and_5_out ? d_ff_75_qn : 1'bz;  // Controlled_Buffer controlled_buffer_177
  assign controlled_buffer_178_out = and_5_out ? controlled_buffer_184_out : 1'bz;  // Controlled_Buffer controlled_buffer_178
  assign controlled_buffer_169_out = and_6_out ? d_ff_76_qn : 1'bz;  // Controlled_Buffer controlled_buffer_179
  assign controlled_buffer_180_out = and_6_out ? controlled_buffer_184_out : 1'bz;  // Controlled_Buffer controlled_buffer_180
  assign controlled_buffer_169_out = and_7_out ? d_ff_77_qn : 1'bz;  // Controlled_Buffer controlled_buffer_181
  assign controlled_buffer_182_out = and_7_out ? controlled_buffer_184_out : 1'bz;  // Controlled_Buffer controlled_buffer_182
  assign controlled_buffer_145_out = nor_6_out ? controlled_buffer_169_out : 1'bz;  // Controlled_Buffer controlled_buffer_183
  assign controlled_buffer_184_out = nor_8_out ? multiplexer_5_out : 1'bz;  // Controlled_Buffer controlled_buffer_184
  D_Flip_Flop #(.trigger("high")) d_ff_78 (
    .clk(1'b1), .D(controlled_buffer_170_out), .Qn(d_ff_78_qn));  // open: Q, preset, en, reset
  assign controlled_buffer_185_out = and_1_out ? d_ff_78_qn : 1'bz;  // Controlled_Buffer controlled_buffer_185
  D_Flip_Flop #(.trigger("high")) d_ff_79 (
    .clk(1'b1), .D(controlled_buffer_172_out), .Qn(d_ff_79_qn));  // open: Q, preset, en, reset
  assign controlled_buffer_185_out = and_2_out ? d_ff_79_qn : 1'bz;  // Controlled_Buffer controlled_buffer_186
  D_Flip_Flop #(.trigger("high")) d_ff_80 (
    .clk(1'b1), .D(controlled_buffer_174_out), .Qn(d_ff_80_qn));  // open: Q, preset, en, reset
  assign controlled_buffer_185_out = and_3_out ? d_ff_80_qn : 1'bz;  // Controlled_Buffer controlled_buffer_187
  D_Flip_Flop #(.trigger("high")) d_ff_81 (
    .clk(1'b1), .D(controlled_buffer_176_out), .Qn(d_ff_81_qn));  // open: Q, preset, en, reset
  assign controlled_buffer_185_out = and_4_out ? d_ff_81_qn : 1'bz;  // Controlled_Buffer controlled_buffer_188
  D_Flip_Flop #(.trigger("high")) d_ff_82 (
    .clk(1'b1), .D(controlled_buffer_178_out), .Qn(d_ff_82_qn));  // open: Q, preset, en, reset
  assign controlled_buffer_185_out = and_5_out ? d_ff_82_qn : 1'bz;  // Controlled_Buffer controlled_buffer_189
  assign controlled_buffer_185_out = and_6_out ? d_ff_83_qn : 1'bz;  // Controlled_Buffer controlled_buffer_190
  D_Flip_Flop #(.trigger("high")) d_ff_83 (
    .clk(1'b1), .D(controlled_buffer_180_out), .Qn(d_ff_83_qn));  // open: Q, preset, en, reset
  D_Flip_Flop #(.trigger("high")) d_ff_84 (
    .clk(1'b1), .D(controlled_buffer_182_out), .Qn(d_ff_84_qn));  // open: Q, preset, en, reset
  assign controlled_buffer_185_out = and_7_out ? d_ff_84_qn : 1'bz;  // Controlled_Buffer controlled_buffer_191
  assign controlled_buffer_145_out = nor_8_out ? controlled_buffer_185_out : 1'bz;  // Controlled_Buffer controlled_buffer_192
  Multiplexer #(.enable("false")) multiplexer_6 (
    .in0(controlled_buffer_145_out), .in1(1'b1), .out(RAM_CB1), .sel(PCLK));
  assign controlled_buffer_193_out = and_1_out ? controlled_buffer_200_out : 1'bz;  // Controlled_Buffer controlled_buffer_193
  assign controlled_buffer_194_out = and_2_out ? controlled_buffer_200_out : 1'bz;  // Controlled_Buffer controlled_buffer_194
  assign controlled_buffer_195_out = and_3_out ? controlled_buffer_200_out : 1'bz;  // Controlled_Buffer controlled_buffer_195
  assign controlled_buffer_196_out = and_4_out ? controlled_buffer_200_out : 1'bz;  // Controlled_Buffer controlled_buffer_196
  assign controlled_buffer_197_out = and_5_out ? controlled_buffer_200_out : 1'bz;  // Controlled_Buffer controlled_buffer_197
  assign controlled_buffer_198_out = and_6_out ? controlled_buffer_200_out : 1'bz;  // Controlled_Buffer controlled_buffer_198
  assign controlled_buffer_199_out = and_7_out ? controlled_buffer_200_out : 1'bz;  // Controlled_Buffer controlled_buffer_199
  assign controlled_buffer_200_out = nor_2_out ? multiplexer_7_out : 1'bz;  // Controlled_Buffer controlled_buffer_200
  D_Flip_Flop #(.trigger("high")) d_ff_85 (
    .clk(1'b1), .D(controlled_buffer_193_out), .Qn(d_ff_85_qn));  // open: Q, preset, en, reset
  assign controlled_buffer_201_out = and_1_out ? d_ff_85_qn : 1'bz;  // Controlled_Buffer controlled_buffer_201
  assign controlled_buffer_201_out = and_2_out ? d_ff_86_qn : 1'bz;  // Controlled_Buffer controlled_buffer_202
  D_Flip_Flop #(.trigger("high")) d_ff_86 (
    .clk(1'b1), .D(controlled_buffer_194_out), .Qn(d_ff_86_qn));  // open: Q, preset, en, reset
  D_Flip_Flop #(.trigger("high")) d_ff_87 (
    .clk(1'b1), .D(controlled_buffer_195_out), .Qn(d_ff_87_qn));  // open: Q, preset, en, reset
  assign controlled_buffer_201_out = and_3_out ? d_ff_87_qn : 1'bz;  // Controlled_Buffer controlled_buffer_203
  D_Flip_Flop #(.trigger("high")) d_ff_88 (
    .clk(1'b1), .D(controlled_buffer_196_out), .Qn(d_ff_88_qn));  // open: Q, preset, en, reset
  assign controlled_buffer_201_out = and_4_out ? d_ff_88_qn : 1'bz;  // Controlled_Buffer controlled_buffer_204
  assign controlled_buffer_201_out = and_5_out ? d_ff_89_qn : 1'bz;  // Controlled_Buffer controlled_buffer_205
  D_Flip_Flop #(.trigger("high")) d_ff_89 (
    .clk(1'b1), .D(controlled_buffer_197_out), .Qn(d_ff_89_qn));  // open: Q, preset, en, reset
  assign controlled_buffer_201_out = and_6_out ? d_ff_90_qn : 1'bz;  // Controlled_Buffer controlled_buffer_206
  D_Flip_Flop #(.trigger("high")) d_ff_90 (
    .clk(1'b1), .D(controlled_buffer_198_out), .Qn(d_ff_90_qn));  // open: Q, preset, en, reset
  D_Flip_Flop #(.trigger("high")) d_ff_91 (
    .clk(1'b1), .D(controlled_buffer_199_out), .Qn(d_ff_91_qn));  // open: Q, preset, en, reset
  assign controlled_buffer_201_out = and_7_out ? d_ff_91_qn : 1'bz;  // Controlled_Buffer controlled_buffer_207
  assign controlled_buffer_208_out = nor_4_out ? multiplexer_7_out : 1'bz;  // Controlled_Buffer controlled_buffer_208
  assign controlled_buffer_209_out = nor_2_out ? controlled_buffer_201_out : 1'bz;  // Controlled_Buffer controlled_buffer_209
  Multiplexer #(.enable("false")) multiplexer_7 (.in0(CB0_RAM), .in1(1'b1), .out(multiplexer_7_out), .sel(PCLK));
  D_Flip_Flop #(.trigger("high")) d_ff_92 (
    .clk(1'b1), .D(controlled_buffer_210_out), .Qn(d_ff_92_qn));  // open: Q, preset, en, reset
  assign controlled_buffer_210_out = and_1_out ? controlled_buffer_208_out : 1'bz;  // Controlled_Buffer controlled_buffer_210
  D_Flip_Flop #(.trigger("high")) d_ff_93 (
    .clk(1'b1), .D(controlled_buffer_211_out), .Qn(d_ff_93_qn));  // open: Q, preset, en, reset
  assign controlled_buffer_211_out = and_2_out ? controlled_buffer_208_out : 1'bz;  // Controlled_Buffer controlled_buffer_211
  D_Flip_Flop #(.trigger("high")) d_ff_94 (
    .clk(1'b1), .D(controlled_buffer_212_out), .Qn(d_ff_94_qn));  // open: Q, preset, en, reset
  assign controlled_buffer_212_out = and_3_out ? controlled_buffer_208_out : 1'bz;  // Controlled_Buffer controlled_buffer_212
  D_Flip_Flop #(.trigger("high")) d_ff_95 (
    .clk(1'b1), .D(controlled_buffer_213_out), .Qn(d_ff_95_qn));  // open: Q, preset, en, reset
  assign controlled_buffer_213_out = and_4_out ? controlled_buffer_208_out : 1'bz;  // Controlled_Buffer controlled_buffer_213
  D_Flip_Flop #(.trigger("high")) d_ff_96 (
    .clk(1'b1), .D(controlled_buffer_214_out), .Qn(d_ff_96_qn));  // open: Q, preset, en, reset
  assign controlled_buffer_214_out = and_5_out ? controlled_buffer_208_out : 1'bz;  // Controlled_Buffer controlled_buffer_214
  D_Flip_Flop #(.trigger("high")) d_ff_97 (
    .clk(1'b1), .D(controlled_buffer_215_out), .Qn(d_ff_97_qn));  // open: Q, preset, en, reset
  assign controlled_buffer_215_out = and_6_out ? controlled_buffer_208_out : 1'bz;  // Controlled_Buffer controlled_buffer_215
  D_Flip_Flop #(.trigger("high")) d_ff_98 (
    .clk(1'b1), .D(controlled_buffer_216_out), .Qn(d_ff_98_qn));  // open: Q, preset, en, reset
  assign controlled_buffer_216_out = and_7_out ? controlled_buffer_208_out : 1'bz;  // Controlled_Buffer controlled_buffer_216
  assign controlled_buffer_217_out = and_1_out ? d_ff_92_qn : 1'bz;  // Controlled_Buffer controlled_buffer_217
  assign controlled_buffer_218_out = and_1_out ? controlled_buffer_231_out : 1'bz;  // Controlled_Buffer controlled_buffer_218
  assign controlled_buffer_217_out = and_2_out ? d_ff_93_qn : 1'bz;  // Controlled_Buffer controlled_buffer_219
  assign controlled_buffer_220_out = and_2_out ? controlled_buffer_231_out : 1'bz;  // Controlled_Buffer controlled_buffer_220
  assign controlled_buffer_217_out = and_3_out ? d_ff_94_qn : 1'bz;  // Controlled_Buffer controlled_buffer_221
  assign controlled_buffer_222_out = and_3_out ? controlled_buffer_231_out : 1'bz;  // Controlled_Buffer controlled_buffer_222
  assign controlled_buffer_217_out = and_4_out ? d_ff_95_qn : 1'bz;  // Controlled_Buffer controlled_buffer_223
  assign controlled_buffer_224_out = and_4_out ? controlled_buffer_231_out : 1'bz;  // Controlled_Buffer controlled_buffer_224
  assign controlled_buffer_217_out = and_5_out ? d_ff_96_qn : 1'bz;  // Controlled_Buffer controlled_buffer_225
  assign controlled_buffer_226_out = and_5_out ? controlled_buffer_231_out : 1'bz;  // Controlled_Buffer controlled_buffer_226
  assign controlled_buffer_217_out = and_6_out ? d_ff_97_qn : 1'bz;  // Controlled_Buffer controlled_buffer_227
  assign controlled_buffer_228_out = and_6_out ? controlled_buffer_231_out : 1'bz;  // Controlled_Buffer controlled_buffer_228
  assign controlled_buffer_217_out = and_7_out ? d_ff_98_qn : 1'bz;  // Controlled_Buffer controlled_buffer_229
  assign controlled_buffer_230_out = and_7_out ? controlled_buffer_231_out : 1'bz;  // Controlled_Buffer controlled_buffer_230
  assign controlled_buffer_231_out = nor_6_out ? multiplexer_7_out : 1'bz;  // Controlled_Buffer controlled_buffer_231
  assign controlled_buffer_209_out = nor_4_out ? controlled_buffer_217_out : 1'bz;  // Controlled_Buffer controlled_buffer_232
  D_Flip_Flop #(.trigger("high")) d_ff_99 (
    .clk(1'b1), .D(controlled_buffer_218_out), .Qn(d_ff_99_qn));  // open: Q, preset, en, reset
  D_Flip_Flop #(.trigger("high")) d_ff_100 (
    .clk(1'b1), .D(controlled_buffer_220_out), .Qn(d_ff_100_qn));  // open: Q, preset, en, reset
  D_Flip_Flop #(.trigger("high")) d_ff_101 (
    .clk(1'b1), .D(controlled_buffer_222_out), .Qn(d_ff_101_qn));  // open: Q, preset, en, reset
  D_Flip_Flop #(.trigger("high")) d_ff_102 (
    .clk(1'b1), .D(controlled_buffer_224_out), .Qn(d_ff_102_qn));  // open: Q, preset, en, reset
  D_Flip_Flop #(.trigger("high")) d_ff_103 (
    .clk(1'b1), .D(controlled_buffer_226_out), .Qn(d_ff_103_qn));  // open: Q, preset, en, reset
  D_Flip_Flop #(.trigger("high")) d_ff_104 (
    .clk(1'b1), .D(controlled_buffer_228_out), .Qn(d_ff_104_qn));  // open: Q, preset, en, reset
  D_Flip_Flop #(.trigger("high")) d_ff_105 (
    .clk(1'b1), .D(controlled_buffer_230_out), .Qn(d_ff_105_qn));  // open: Q, preset, en, reset
  assign controlled_buffer_233_out = and_1_out ? d_ff_99_qn : 1'bz;  // Controlled_Buffer controlled_buffer_233
  assign controlled_buffer_234_out = and_1_out ? controlled_buffer_248_out : 1'bz;  // Controlled_Buffer controlled_buffer_234
  assign controlled_buffer_233_out = and_2_out ? d_ff_100_qn : 1'bz;  // Controlled_Buffer controlled_buffer_235
  assign controlled_buffer_236_out = and_2_out ? controlled_buffer_248_out : 1'bz;  // Controlled_Buffer controlled_buffer_236
  assign controlled_buffer_233_out = and_3_out ? d_ff_101_qn : 1'bz;  // Controlled_Buffer controlled_buffer_237
  assign controlled_buffer_238_out = and_3_out ? controlled_buffer_248_out : 1'bz;  // Controlled_Buffer controlled_buffer_238
  assign controlled_buffer_233_out = and_4_out ? d_ff_102_qn : 1'bz;  // Controlled_Buffer controlled_buffer_239
  assign controlled_buffer_240_out = and_4_out ? controlled_buffer_248_out : 1'bz;  // Controlled_Buffer controlled_buffer_240
  assign controlled_buffer_233_out = and_5_out ? d_ff_103_qn : 1'bz;  // Controlled_Buffer controlled_buffer_241
  assign controlled_buffer_242_out = and_5_out ? controlled_buffer_248_out : 1'bz;  // Controlled_Buffer controlled_buffer_242
  assign controlled_buffer_233_out = and_6_out ? d_ff_104_qn : 1'bz;  // Controlled_Buffer controlled_buffer_243
  assign controlled_buffer_244_out = and_6_out ? controlled_buffer_248_out : 1'bz;  // Controlled_Buffer controlled_buffer_244
  assign controlled_buffer_233_out = and_7_out ? d_ff_105_qn : 1'bz;  // Controlled_Buffer controlled_buffer_245
  assign controlled_buffer_246_out = and_7_out ? controlled_buffer_248_out : 1'bz;  // Controlled_Buffer controlled_buffer_246
  assign controlled_buffer_209_out = nor_6_out ? controlled_buffer_233_out : 1'bz;  // Controlled_Buffer controlled_buffer_247
  assign controlled_buffer_248_out = nor_8_out ? multiplexer_7_out : 1'bz;  // Controlled_Buffer controlled_buffer_248
  assign controlled_buffer_249_out = and_1_out ? d_ff_106_qn : 1'bz;  // Controlled_Buffer controlled_buffer_249
  D_Flip_Flop #(.trigger("high")) d_ff_106 (
    .clk(1'b1), .D(controlled_buffer_234_out), .Qn(d_ff_106_qn));  // open: Q, preset, en, reset
  D_Flip_Flop #(.trigger("high")) d_ff_107 (
    .clk(1'b1), .D(controlled_buffer_236_out), .Qn(d_ff_107_qn));  // open: Q, preset, en, reset
  assign controlled_buffer_249_out = and_2_out ? d_ff_107_qn : 1'bz;  // Controlled_Buffer controlled_buffer_250
  D_Flip_Flop #(.trigger("high")) d_ff_108 (
    .clk(1'b1), .D(controlled_buffer_238_out), .Qn(d_ff_108_qn));  // open: Q, preset, en, reset
  assign controlled_buffer_249_out = and_3_out ? d_ff_108_qn : 1'bz;  // Controlled_Buffer controlled_buffer_251
  D_Flip_Flop #(.trigger("high")) d_ff_109 (
    .clk(1'b1), .D(controlled_buffer_240_out), .Qn(d_ff_109_qn));  // open: Q, preset, en, reset
  assign controlled_buffer_249_out = and_4_out ? d_ff_109_qn : 1'bz;  // Controlled_Buffer controlled_buffer_252
  D_Flip_Flop #(.trigger("high")) d_ff_110 (
    .clk(1'b1), .D(controlled_buffer_242_out), .Qn(d_ff_110_qn));  // open: Q, preset, en, reset
  assign controlled_buffer_249_out = and_5_out ? d_ff_110_qn : 1'bz;  // Controlled_Buffer controlled_buffer_253
  D_Flip_Flop #(.trigger("high")) d_ff_111 (
    .clk(1'b1), .D(controlled_buffer_244_out), .Qn(d_ff_111_qn));  // open: Q, preset, en, reset
  assign controlled_buffer_249_out = and_6_out ? d_ff_111_qn : 1'bz;  // Controlled_Buffer controlled_buffer_254
  D_Flip_Flop #(.trigger("high")) d_ff_112 (
    .clk(1'b1), .D(controlled_buffer_246_out), .Qn(d_ff_112_qn));  // open: Q, preset, en, reset
  assign controlled_buffer_249_out = and_7_out ? d_ff_112_qn : 1'bz;  // Controlled_Buffer controlled_buffer_255
  assign controlled_buffer_209_out = nor_8_out ? controlled_buffer_249_out : 1'bz;  // Controlled_Buffer controlled_buffer_256
  Multiplexer #(.enable("false")) multiplexer_8 (
    .in0(controlled_buffer_209_out), .in1(1'b1), .out(RAM_CB0), .sel(PCLK));
  assign controlled_buffer_257_out = nor_2_out ? multiplexer_9_out : 1'bz;  // Controlled_Buffer controlled_buffer_257
  assign controlled_buffer_258_out = and_1_out ? controlled_buffer_257_out : 1'bz;  // Controlled_Buffer controlled_buffer_258
  assign controlled_buffer_259_out = and_2_out ? controlled_buffer_257_out : 1'bz;  // Controlled_Buffer controlled_buffer_259
  assign controlled_buffer_260_out = and_3_out ? controlled_buffer_257_out : 1'bz;  // Controlled_Buffer controlled_buffer_260
  assign controlled_buffer_261_out = and_4_out ? controlled_buffer_257_out : 1'bz;  // Controlled_Buffer controlled_buffer_261
  assign controlled_buffer_262_out = and_5_out ? controlled_buffer_257_out : 1'bz;  // Controlled_Buffer controlled_buffer_262
  assign controlled_buffer_263_out = and_6_out ? controlled_buffer_257_out : 1'bz;  // Controlled_Buffer controlled_buffer_263
  assign controlled_buffer_264_out = and_7_out ? controlled_buffer_257_out : 1'bz;  // Controlled_Buffer controlled_buffer_264
  Multiplexer #(.enable("false")) multiplexer_9 (.in0(CY1_RAM), .in1(1'b1), .out(multiplexer_9_out), .sel(PCLK));
  D_Flip_Flop #(.trigger("high")) d_ff_113 (
    .clk(1'b1), .D(controlled_buffer_258_out), .Qn(d_ff_113_qn));  // open: Q, preset, en, reset
  assign controlled_buffer_265_out = and_1_out ? d_ff_113_qn : 1'bz;  // Controlled_Buffer controlled_buffer_265
  assign controlled_buffer_266_out = and_1_out ? controlled_buffer_280_out : 1'bz;  // Controlled_Buffer controlled_buffer_266
  D_Flip_Flop #(.trigger("high")) d_ff_114 (
    .clk(1'b1), .D(controlled_buffer_259_out), .Qn(d_ff_114_qn));  // open: Q, preset, en, reset
  assign controlled_buffer_265_out = and_2_out ? d_ff_114_qn : 1'bz;  // Controlled_Buffer controlled_buffer_267
  assign controlled_buffer_268_out = and_2_out ? controlled_buffer_280_out : 1'bz;  // Controlled_Buffer controlled_buffer_268
  D_Flip_Flop #(.trigger("high")) d_ff_115 (
    .clk(1'b1), .D(controlled_buffer_260_out), .Qn(d_ff_115_qn));  // open: Q, preset, en, reset
  assign controlled_buffer_265_out = and_3_out ? d_ff_115_qn : 1'bz;  // Controlled_Buffer controlled_buffer_269
  assign controlled_buffer_270_out = and_3_out ? controlled_buffer_280_out : 1'bz;  // Controlled_Buffer controlled_buffer_270
  assign controlled_buffer_265_out = and_4_out ? d_ff_116_qn : 1'bz;  // Controlled_Buffer controlled_buffer_271
  D_Flip_Flop #(.trigger("high")) d_ff_116 (
    .clk(1'b1), .D(controlled_buffer_261_out), .Qn(d_ff_116_qn));  // open: Q, preset, en, reset
  assign controlled_buffer_272_out = and_4_out ? controlled_buffer_280_out : 1'bz;  // Controlled_Buffer controlled_buffer_272
  D_Flip_Flop #(.trigger("high")) d_ff_117 (
    .clk(1'b1), .D(controlled_buffer_262_out), .Qn(d_ff_117_qn));  // open: Q, preset, en, reset
  assign controlled_buffer_265_out = and_5_out ? d_ff_117_qn : 1'bz;  // Controlled_Buffer controlled_buffer_273
  assign controlled_buffer_274_out = and_5_out ? controlled_buffer_280_out : 1'bz;  // Controlled_Buffer controlled_buffer_274
  D_Flip_Flop #(.trigger("high")) d_ff_118 (
    .clk(1'b1), .D(controlled_buffer_263_out), .Qn(d_ff_118_qn));  // open: Q, preset, en, reset
  assign controlled_buffer_265_out = and_6_out ? d_ff_118_qn : 1'bz;  // Controlled_Buffer controlled_buffer_275
  assign controlled_buffer_276_out = and_6_out ? controlled_buffer_280_out : 1'bz;  // Controlled_Buffer controlled_buffer_276
  assign controlled_buffer_265_out = and_7_out ? d_ff_119_qn : 1'bz;  // Controlled_Buffer controlled_buffer_277
  D_Flip_Flop #(.trigger("high")) d_ff_119 (
    .clk(1'b1), .D(controlled_buffer_264_out), .Qn(d_ff_119_qn));  // open: Q, preset, en, reset
  assign controlled_buffer_278_out = and_7_out ? controlled_buffer_280_out : 1'bz;  // Controlled_Buffer controlled_buffer_278
  assign controlled_buffer_279_out = nor_2_out ? controlled_buffer_265_out : 1'bz;  // Controlled_Buffer controlled_buffer_279
  assign controlled_buffer_280_out = nor_4_out ? multiplexer_9_out : 1'bz;  // Controlled_Buffer controlled_buffer_280
  D_Flip_Flop #(.trigger("high")) d_ff_120 (
    .clk(1'b1), .D(controlled_buffer_266_out), .Qn(d_ff_120_qn));  // open: Q, preset, en, reset
  D_Flip_Flop #(.trigger("high")) d_ff_121 (
    .clk(1'b1), .D(controlled_buffer_268_out), .Qn(d_ff_121_qn));  // open: Q, preset, en, reset
  D_Flip_Flop #(.trigger("high")) d_ff_122 (
    .clk(1'b1), .D(controlled_buffer_270_out), .Qn(d_ff_122_qn));  // open: Q, preset, en, reset
  D_Flip_Flop #(.trigger("high")) d_ff_123 (
    .clk(1'b1), .D(controlled_buffer_272_out), .Qn(d_ff_123_qn));  // open: Q, preset, en, reset
  D_Flip_Flop #(.trigger("high")) d_ff_124 (
    .clk(1'b1), .D(controlled_buffer_274_out), .Qn(d_ff_124_qn));  // open: Q, preset, en, reset
  D_Flip_Flop #(.trigger("high")) d_ff_125 (
    .clk(1'b1), .D(controlled_buffer_276_out), .Qn(d_ff_125_qn));  // open: Q, preset, en, reset
  D_Flip_Flop #(.trigger("high")) d_ff_126 (
    .clk(1'b1), .D(controlled_buffer_278_out), .Qn(d_ff_126_qn));  // open: Q, preset, en, reset
  assign controlled_buffer_281_out = and_1_out ? d_ff_120_qn : 1'bz;  // Controlled_Buffer controlled_buffer_281
  assign controlled_buffer_282_out = and_1_out ? controlled_buffer_295_out : 1'bz;  // Controlled_Buffer controlled_buffer_282
  assign controlled_buffer_281_out = and_2_out ? d_ff_121_qn : 1'bz;  // Controlled_Buffer controlled_buffer_283
  assign controlled_buffer_284_out = and_2_out ? controlled_buffer_295_out : 1'bz;  // Controlled_Buffer controlled_buffer_284
  assign controlled_buffer_281_out = and_3_out ? d_ff_122_qn : 1'bz;  // Controlled_Buffer controlled_buffer_285
  assign controlled_buffer_286_out = and_3_out ? controlled_buffer_295_out : 1'bz;  // Controlled_Buffer controlled_buffer_286
  assign controlled_buffer_281_out = and_4_out ? d_ff_123_qn : 1'bz;  // Controlled_Buffer controlled_buffer_287
  assign controlled_buffer_288_out = and_4_out ? controlled_buffer_295_out : 1'bz;  // Controlled_Buffer controlled_buffer_288
  assign controlled_buffer_281_out = and_5_out ? d_ff_124_qn : 1'bz;  // Controlled_Buffer controlled_buffer_289
  assign controlled_buffer_290_out = and_5_out ? controlled_buffer_295_out : 1'bz;  // Controlled_Buffer controlled_buffer_290
  assign controlled_buffer_281_out = and_6_out ? d_ff_125_qn : 1'bz;  // Controlled_Buffer controlled_buffer_291
  assign controlled_buffer_292_out = and_6_out ? controlled_buffer_295_out : 1'bz;  // Controlled_Buffer controlled_buffer_292
  assign controlled_buffer_281_out = and_7_out ? d_ff_126_qn : 1'bz;  // Controlled_Buffer controlled_buffer_293
  assign controlled_buffer_294_out = and_7_out ? controlled_buffer_295_out : 1'bz;  // Controlled_Buffer controlled_buffer_294
  assign controlled_buffer_295_out = nor_6_out ? multiplexer_9_out : 1'bz;  // Controlled_Buffer controlled_buffer_295
  assign controlled_buffer_279_out = nor_4_out ? controlled_buffer_281_out : 1'bz;  // Controlled_Buffer controlled_buffer_296
  D_Flip_Flop #(.trigger("high")) d_ff_127 (
    .clk(1'b1), .D(controlled_buffer_282_out), .Qn(d_ff_127_qn));  // open: Q, preset, en, reset
  assign controlled_buffer_297_out = and_1_out ? d_ff_127_qn : 1'bz;  // Controlled_Buffer controlled_buffer_297
  D_Flip_Flop #(.trigger("high")) d_ff_128 (
    .clk(1'b1), .D(controlled_buffer_284_out), .Qn(d_ff_128_qn));  // open: Q, preset, en, reset
  assign controlled_buffer_297_out = and_2_out ? d_ff_128_qn : 1'bz;  // Controlled_Buffer controlled_buffer_298
  assign controlled_buffer_297_out = and_3_out ? d_ff_129_qn : 1'bz;  // Controlled_Buffer controlled_buffer_299
  D_Flip_Flop #(.trigger("high")) d_ff_129 (
    .clk(1'b1), .D(controlled_buffer_286_out), .Qn(d_ff_129_qn));  // open: Q, preset, en, reset
  assign controlled_buffer_297_out = and_4_out ? d_ff_130_qn : 1'bz;  // Controlled_Buffer controlled_buffer_300
  D_Flip_Flop #(.trigger("high")) d_ff_130 (
    .clk(1'b1), .D(controlled_buffer_288_out), .Qn(d_ff_130_qn));  // open: Q, preset, en, reset
  D_Flip_Flop #(.trigger("high")) d_ff_131 (
    .clk(1'b1), .D(controlled_buffer_290_out), .Qn(d_ff_131_qn));  // open: Q, preset, en, reset
  assign controlled_buffer_297_out = and_5_out ? d_ff_131_qn : 1'bz;  // Controlled_Buffer controlled_buffer_301
  assign controlled_buffer_297_out = and_6_out ? d_ff_132_qn : 1'bz;  // Controlled_Buffer controlled_buffer_302
  D_Flip_Flop #(.trigger("high")) d_ff_132 (
    .clk(1'b1), .D(controlled_buffer_292_out), .Qn(d_ff_132_qn));  // open: Q, preset, en, reset
  D_Flip_Flop #(.trigger("high")) d_ff_133 (
    .clk(1'b1), .D(controlled_buffer_294_out), .Qn(d_ff_133_qn));  // open: Q, preset, en, reset
  assign controlled_buffer_297_out = and_7_out ? d_ff_133_qn : 1'bz;  // Controlled_Buffer controlled_buffer_303
  assign controlled_buffer_279_out = nor_6_out ? controlled_buffer_297_out : 1'bz;  // Controlled_Buffer controlled_buffer_304
  assign controlled_buffer_305_out = nor_8_out ? multiplexer_9_out : 1'bz;  // Controlled_Buffer controlled_buffer_305
  assign controlled_buffer_306_out = and_1_out ? controlled_buffer_305_out : 1'bz;  // Controlled_Buffer controlled_buffer_306
  assign controlled_buffer_307_out = and_2_out ? controlled_buffer_305_out : 1'bz;  // Controlled_Buffer controlled_buffer_307
  assign controlled_buffer_308_out = and_3_out ? controlled_buffer_305_out : 1'bz;  // Controlled_Buffer controlled_buffer_308
  assign controlled_buffer_309_out = and_4_out ? controlled_buffer_305_out : 1'bz;  // Controlled_Buffer controlled_buffer_309
  assign controlled_buffer_310_out = and_5_out ? controlled_buffer_305_out : 1'bz;  // Controlled_Buffer controlled_buffer_310
  assign controlled_buffer_311_out = and_6_out ? controlled_buffer_305_out : 1'bz;  // Controlled_Buffer controlled_buffer_311
  assign controlled_buffer_312_out = and_7_out ? controlled_buffer_305_out : 1'bz;  // Controlled_Buffer controlled_buffer_312
  assign controlled_buffer_313_out = and_1_out ? d_ff_134_qn : 1'bz;  // Controlled_Buffer controlled_buffer_313
  D_Flip_Flop #(.trigger("high")) d_ff_134 (
    .clk(1'b1), .D(controlled_buffer_306_out), .Qn(d_ff_134_qn));  // open: Q, preset, en, reset
  assign controlled_buffer_313_out = and_2_out ? d_ff_135_qn : 1'bz;  // Controlled_Buffer controlled_buffer_314
  D_Flip_Flop #(.trigger("high")) d_ff_135 (
    .clk(1'b1), .D(controlled_buffer_307_out), .Qn(d_ff_135_qn));  // open: Q, preset, en, reset
  D_Flip_Flop #(.trigger("high")) d_ff_136 (
    .clk(1'b1), .D(controlled_buffer_308_out), .Qn(d_ff_136_qn));  // open: Q, preset, en, reset
  assign controlled_buffer_313_out = and_3_out ? d_ff_136_qn : 1'bz;  // Controlled_Buffer controlled_buffer_315
  D_Flip_Flop #(.trigger("high")) d_ff_137 (
    .clk(1'b1), .D(controlled_buffer_309_out), .Qn(d_ff_137_qn));  // open: Q, preset, en, reset
  assign controlled_buffer_313_out = and_4_out ? d_ff_137_qn : 1'bz;  // Controlled_Buffer controlled_buffer_316
  assign controlled_buffer_313_out = and_5_out ? d_ff_138_qn : 1'bz;  // Controlled_Buffer controlled_buffer_317
  D_Flip_Flop #(.trigger("high")) d_ff_138 (
    .clk(1'b1), .D(controlled_buffer_310_out), .Qn(d_ff_138_qn));  // open: Q, preset, en, reset
  D_Flip_Flop #(.trigger("high")) d_ff_139 (
    .clk(1'b1), .D(controlled_buffer_311_out), .Qn(d_ff_139_qn));  // open: Q, preset, en, reset
  assign controlled_buffer_313_out = and_6_out ? d_ff_139_qn : 1'bz;  // Controlled_Buffer controlled_buffer_318
  D_Flip_Flop #(.trigger("high")) d_ff_140 (
    .clk(1'b1), .D(controlled_buffer_312_out), .Qn(d_ff_140_qn));  // open: Q, preset, en, reset
  assign controlled_buffer_313_out = and_7_out ? d_ff_140_qn : 1'bz;  // Controlled_Buffer controlled_buffer_319
  assign controlled_buffer_279_out = nor_8_out ? controlled_buffer_313_out : 1'bz;  // Controlled_Buffer controlled_buffer_320
  Multiplexer #(.enable("false")) multiplexer_10 (
    .in0(controlled_buffer_279_out), .in1(1'b1), .out(RAM_CY1), .sel(PCLK));
  assign controlled_buffer_321_out = nor_2_out ? multiplexer_11_out : 1'bz;  // Controlled_Buffer controlled_buffer_321
  D_Flip_Flop #(.trigger("high")) d_ff_141 (
    .clk(1'b1), .D(controlled_buffer_322_out), .Qn(d_ff_141_qn));  // open: Q, preset, en, reset
  assign controlled_buffer_322_out = and_1_out ? controlled_buffer_321_out : 1'bz;  // Controlled_Buffer controlled_buffer_322
  D_Flip_Flop #(.trigger("high")) d_ff_142 (
    .clk(1'b1), .D(controlled_buffer_323_out), .Qn(d_ff_142_qn));  // open: Q, preset, en, reset
  assign controlled_buffer_323_out = and_2_out ? controlled_buffer_321_out : 1'bz;  // Controlled_Buffer controlled_buffer_323
  D_Flip_Flop #(.trigger("high")) d_ff_143 (
    .clk(1'b1), .D(controlled_buffer_324_out), .Qn(d_ff_143_qn));  // open: Q, preset, en, reset
  assign controlled_buffer_324_out = and_3_out ? controlled_buffer_321_out : 1'bz;  // Controlled_Buffer controlled_buffer_324
  D_Flip_Flop #(.trigger("high")) d_ff_144 (
    .clk(1'b1), .D(controlled_buffer_325_out), .Qn(d_ff_144_qn));  // open: Q, preset, en, reset
  assign controlled_buffer_325_out = and_4_out ? controlled_buffer_321_out : 1'bz;  // Controlled_Buffer controlled_buffer_325
  D_Flip_Flop #(.trigger("high")) d_ff_145 (
    .clk(1'b1), .D(controlled_buffer_326_out), .Qn(d_ff_145_qn));  // open: Q, preset, en, reset
  assign controlled_buffer_326_out = and_5_out ? controlled_buffer_321_out : 1'bz;  // Controlled_Buffer controlled_buffer_326
  D_Flip_Flop #(.trigger("high")) d_ff_146 (
    .clk(1'b1), .D(controlled_buffer_327_out), .Qn(d_ff_146_qn));  // open: Q, preset, en, reset
  assign controlled_buffer_327_out = and_6_out ? controlled_buffer_321_out : 1'bz;  // Controlled_Buffer controlled_buffer_327
  D_Flip_Flop #(.trigger("high")) d_ff_147 (
    .clk(1'b1), .D(controlled_buffer_328_out), .Qn(d_ff_147_qn));  // open: Q, preset, en, reset
  assign controlled_buffer_328_out = and_7_out ? controlled_buffer_321_out : 1'bz;  // Controlled_Buffer controlled_buffer_328
  assign controlled_buffer_329_out = and_1_out ? d_ff_141_qn : 1'bz;  // Controlled_Buffer controlled_buffer_329
  assign controlled_buffer_330_out = and_1_out ? controlled_buffer_344_out : 1'bz;  // Controlled_Buffer controlled_buffer_330
  assign controlled_buffer_329_out = and_2_out ? d_ff_142_qn : 1'bz;  // Controlled_Buffer controlled_buffer_331
  assign controlled_buffer_332_out = and_2_out ? controlled_buffer_344_out : 1'bz;  // Controlled_Buffer controlled_buffer_332
  assign controlled_buffer_329_out = and_3_out ? d_ff_143_qn : 1'bz;  // Controlled_Buffer controlled_buffer_333
  assign controlled_buffer_334_out = and_3_out ? controlled_buffer_344_out : 1'bz;  // Controlled_Buffer controlled_buffer_334
  assign controlled_buffer_329_out = and_4_out ? d_ff_144_qn : 1'bz;  // Controlled_Buffer controlled_buffer_335
  assign controlled_buffer_336_out = and_4_out ? controlled_buffer_344_out : 1'bz;  // Controlled_Buffer controlled_buffer_336
  assign controlled_buffer_329_out = and_5_out ? d_ff_145_qn : 1'bz;  // Controlled_Buffer controlled_buffer_337
  assign controlled_buffer_338_out = and_5_out ? controlled_buffer_344_out : 1'bz;  // Controlled_Buffer controlled_buffer_338
  assign controlled_buffer_329_out = and_6_out ? d_ff_146_qn : 1'bz;  // Controlled_Buffer controlled_buffer_339
  assign controlled_buffer_340_out = and_6_out ? controlled_buffer_344_out : 1'bz;  // Controlled_Buffer controlled_buffer_340
  assign controlled_buffer_329_out = and_7_out ? d_ff_147_qn : 1'bz;  // Controlled_Buffer controlled_buffer_341
  assign controlled_buffer_342_out = and_7_out ? controlled_buffer_344_out : 1'bz;  // Controlled_Buffer controlled_buffer_342
  assign controlled_buffer_343_out = nor_2_out ? controlled_buffer_329_out : 1'bz;  // Controlled_Buffer controlled_buffer_343
  assign controlled_buffer_344_out = nor_4_out ? multiplexer_11_out : 1'bz;  // Controlled_Buffer controlled_buffer_344
  Multiplexer #(.enable("false")) multiplexer_11 (.in0(CY0_RAM), .in1(1'b1), .out(multiplexer_11_out), .sel(PCLK));
  assign controlled_buffer_345_out = and_1_out ? d_ff_148_qn : 1'bz;  // Controlled_Buffer controlled_buffer_345
  D_Flip_Flop #(.trigger("high")) d_ff_148 (
    .clk(1'b1), .D(controlled_buffer_330_out), .Qn(d_ff_148_qn));  // open: Q, preset, en, reset
  D_Flip_Flop #(.trigger("high")) d_ff_149 (
    .clk(1'b1), .D(controlled_buffer_332_out), .Qn(d_ff_149_qn));  // open: Q, preset, en, reset
  assign controlled_buffer_345_out = and_2_out ? d_ff_149_qn : 1'bz;  // Controlled_Buffer controlled_buffer_346
  D_Flip_Flop #(.trigger("high")) d_ff_150 (
    .clk(1'b1), .D(controlled_buffer_334_out), .Qn(d_ff_150_qn));  // open: Q, preset, en, reset
  assign controlled_buffer_345_out = and_3_out ? d_ff_150_qn : 1'bz;  // Controlled_Buffer controlled_buffer_347
  assign controlled_buffer_345_out = and_4_out ? d_ff_151_qn : 1'bz;  // Controlled_Buffer controlled_buffer_348
  D_Flip_Flop #(.trigger("high")) d_ff_151 (
    .clk(1'b1), .D(controlled_buffer_336_out), .Qn(d_ff_151_qn));  // open: Q, preset, en, reset
  D_Flip_Flop #(.trigger("high")) d_ff_152 (
    .clk(1'b1), .D(controlled_buffer_338_out), .Qn(d_ff_152_qn));  // open: Q, preset, en, reset
  assign controlled_buffer_345_out = and_5_out ? d_ff_152_qn : 1'bz;  // Controlled_Buffer controlled_buffer_349
  D_Flip_Flop #(.trigger("high")) d_ff_153 (
    .clk(1'b1), .D(controlled_buffer_340_out), .Qn(d_ff_153_qn));  // open: Q, preset, en, reset
  assign controlled_buffer_345_out = and_6_out ? d_ff_153_qn : 1'bz;  // Controlled_Buffer controlled_buffer_350
  D_Flip_Flop #(.trigger("high")) d_ff_154 (
    .clk(1'b1), .D(controlled_buffer_342_out), .Qn(d_ff_154_qn));  // open: Q, preset, en, reset
  assign controlled_buffer_345_out = and_7_out ? d_ff_154_qn : 1'bz;  // Controlled_Buffer controlled_buffer_351
  assign controlled_buffer_343_out = nor_4_out ? controlled_buffer_345_out : 1'bz;  // Controlled_Buffer controlled_buffer_352
  assign controlled_buffer_353_out = and_1_out ? controlled_buffer_360_out : 1'bz;  // Controlled_Buffer controlled_buffer_353
  assign controlled_buffer_354_out = and_2_out ? controlled_buffer_360_out : 1'bz;  // Controlled_Buffer controlled_buffer_354
  assign controlled_buffer_355_out = and_3_out ? controlled_buffer_360_out : 1'bz;  // Controlled_Buffer controlled_buffer_355
  assign controlled_buffer_356_out = and_4_out ? controlled_buffer_360_out : 1'bz;  // Controlled_Buffer controlled_buffer_356
  assign controlled_buffer_357_out = and_5_out ? controlled_buffer_360_out : 1'bz;  // Controlled_Buffer controlled_buffer_357
  assign controlled_buffer_358_out = and_6_out ? controlled_buffer_360_out : 1'bz;  // Controlled_Buffer controlled_buffer_358
  assign controlled_buffer_359_out = and_7_out ? controlled_buffer_360_out : 1'bz;  // Controlled_Buffer controlled_buffer_359
  assign controlled_buffer_360_out = nor_6_out ? multiplexer_11_out : 1'bz;  // Controlled_Buffer controlled_buffer_360
  assign controlled_buffer_361_out = and_1_out ? d_ff_155_qn : 1'bz;  // Controlled_Buffer controlled_buffer_361
  D_Flip_Flop #(.trigger("high")) d_ff_155 (
    .clk(1'b1), .D(controlled_buffer_353_out), .Qn(d_ff_155_qn));  // open: Q, preset, en, reset
  D_Flip_Flop #(.trigger("high")) d_ff_156 (
    .clk(1'b1), .D(controlled_buffer_354_out), .Qn(d_ff_156_qn));  // open: Q, preset, en, reset
  assign controlled_buffer_361_out = and_2_out ? d_ff_156_qn : 1'bz;  // Controlled_Buffer controlled_buffer_362
  assign controlled_buffer_361_out = and_3_out ? d_ff_157_qn : 1'bz;  // Controlled_Buffer controlled_buffer_363
  D_Flip_Flop #(.trigger("high")) d_ff_157 (
    .clk(1'b1), .D(controlled_buffer_355_out), .Qn(d_ff_157_qn));  // open: Q, preset, en, reset
  assign controlled_buffer_361_out = and_4_out ? d_ff_158_qn : 1'bz;  // Controlled_Buffer controlled_buffer_364
  D_Flip_Flop #(.trigger("high")) d_ff_158 (
    .clk(1'b1), .D(controlled_buffer_356_out), .Qn(d_ff_158_qn));  // open: Q, preset, en, reset
  D_Flip_Flop #(.trigger("high")) d_ff_159 (
    .clk(1'b1), .D(controlled_buffer_357_out), .Qn(d_ff_159_qn));  // open: Q, preset, en, reset
  assign controlled_buffer_361_out = and_5_out ? d_ff_159_qn : 1'bz;  // Controlled_Buffer controlled_buffer_365
  assign controlled_buffer_361_out = and_6_out ? d_ff_160_qn : 1'bz;  // Controlled_Buffer controlled_buffer_366
  D_Flip_Flop #(.trigger("high")) d_ff_160 (
    .clk(1'b1), .D(controlled_buffer_358_out), .Qn(d_ff_160_qn));  // open: Q, preset, en, reset
  assign controlled_buffer_361_out = and_7_out ? d_ff_161_qn : 1'bz;  // Controlled_Buffer controlled_buffer_367
  D_Flip_Flop #(.trigger("high")) d_ff_161 (
    .clk(1'b1), .D(controlled_buffer_359_out), .Qn(d_ff_161_qn));  // open: Q, preset, en, reset
  assign controlled_buffer_343_out = nor_6_out ? controlled_buffer_361_out : 1'bz;  // Controlled_Buffer controlled_buffer_368
  assign controlled_buffer_369_out = nor_8_out ? multiplexer_11_out : 1'bz;  // Controlled_Buffer controlled_buffer_369
  D_Flip_Flop #(.trigger("high")) d_ff_162 (
    .clk(1'b1), .D(controlled_buffer_370_out), .Qn(d_ff_162_qn));  // open: Q, preset, en, reset
  assign controlled_buffer_370_out = and_1_out ? controlled_buffer_369_out : 1'bz;  // Controlled_Buffer controlled_buffer_370
  D_Flip_Flop #(.trigger("high")) d_ff_163 (
    .clk(1'b1), .D(controlled_buffer_371_out), .Qn(d_ff_163_qn));  // open: Q, preset, en, reset
  assign controlled_buffer_371_out = and_2_out ? controlled_buffer_369_out : 1'bz;  // Controlled_Buffer controlled_buffer_371
  D_Flip_Flop #(.trigger("high")) d_ff_164 (
    .clk(1'b1), .D(controlled_buffer_372_out), .Qn(d_ff_164_qn));  // open: Q, preset, en, reset
  assign controlled_buffer_372_out = and_3_out ? controlled_buffer_369_out : 1'bz;  // Controlled_Buffer controlled_buffer_372
  D_Flip_Flop #(.trigger("high")) d_ff_165 (
    .clk(1'b1), .D(controlled_buffer_373_out), .Qn(d_ff_165_qn));  // open: Q, preset, en, reset
  assign controlled_buffer_373_out = and_4_out ? controlled_buffer_369_out : 1'bz;  // Controlled_Buffer controlled_buffer_373
  D_Flip_Flop #(.trigger("high")) d_ff_166 (
    .clk(1'b1), .D(controlled_buffer_374_out), .Qn(d_ff_166_qn));  // open: Q, preset, en, reset
  assign controlled_buffer_374_out = and_5_out ? controlled_buffer_369_out : 1'bz;  // Controlled_Buffer controlled_buffer_374
  D_Flip_Flop #(.trigger("high")) d_ff_167 (
    .clk(1'b1), .D(controlled_buffer_375_out), .Qn(d_ff_167_qn));  // open: Q, preset, en, reset
  assign controlled_buffer_375_out = and_6_out ? controlled_buffer_369_out : 1'bz;  // Controlled_Buffer controlled_buffer_375
  D_Flip_Flop #(.trigger("high")) d_ff_168 (
    .clk(1'b1), .D(controlled_buffer_376_out), .Qn(d_ff_168_qn));  // open: Q, preset, en, reset
  assign controlled_buffer_376_out = and_7_out ? controlled_buffer_369_out : 1'bz;  // Controlled_Buffer controlled_buffer_376
  assign controlled_buffer_377_out = and_1_out ? d_ff_162_qn : 1'bz;  // Controlled_Buffer controlled_buffer_377
  assign controlled_buffer_377_out = and_2_out ? d_ff_163_qn : 1'bz;  // Controlled_Buffer controlled_buffer_378
  assign controlled_buffer_377_out = and_3_out ? d_ff_164_qn : 1'bz;  // Controlled_Buffer controlled_buffer_379
  assign controlled_buffer_377_out = and_4_out ? d_ff_165_qn : 1'bz;  // Controlled_Buffer controlled_buffer_380
  assign controlled_buffer_377_out = and_5_out ? d_ff_166_qn : 1'bz;  // Controlled_Buffer controlled_buffer_381
  assign controlled_buffer_377_out = and_6_out ? d_ff_167_qn : 1'bz;  // Controlled_Buffer controlled_buffer_382
  assign controlled_buffer_377_out = and_7_out ? d_ff_168_qn : 1'bz;  // Controlled_Buffer controlled_buffer_383
  assign controlled_buffer_343_out = nor_8_out ? controlled_buffer_377_out : 1'bz;  // Controlled_Buffer controlled_buffer_384
  Multiplexer #(.enable("false")) multiplexer_12 (
    .in0(controlled_buffer_343_out), .in1(1'b1), .out(RAM_CY0), .sel(PCLK));

  // Notes on the sheet:
  //   11
  //   10
  //   01
  //   00
endmodule

module COLOR_CONTROL (
  input  PCLK,
  input  DB_PAR,
  input  TH_MUX,
  input  nR7,
  input  nDBE,
  input  PICTURE,
  input  BW,
  output DB_CB,
  output CB_DB,
  output COLOR_EN
);

  wire d_latch_1_q, nand_2_out, nor_1_out, not_1_out, not_3_out;

  D_latch d_latch_1 (.EN(PCLK), .D(DB_PAR), .Q(d_latch_1_q));  // open: NOT_Q
  not not_1 (not_1_out, TH_MUX);
  not not_2 (CB_DB, nor_1_out);
  nor nor_1 (nor_1_out, not_1_out, nR7, nDBE);
  not not_3 (not_3_out, BW);
  nand nand_1 (DB_CB, d_latch_1_q, TH_MUX);
  nand nand_2 (nand_2_out, CB_DB, PICTURE);
  and and_1 (COLOR_EN, nand_2_out, not_3_out);
endmodule

module CONTROL_REGS (
  input  DB0,
  input  DB1,
  input  DB2,
  input  DB3,
  input  DB4,
  input  DB5,
  input  DB6,
  input  DB7,
  input  nDBE,
  input  nW0,
  input  RC,
  input  nW1,
  input  PCLK,
  input  nVIS,
  input  CLIP_B,
  input  CLIP_O,
  output I1_32,
  output OBSEL,
  output BGSEL,
  output O8_16,
  output nSLAVE,
  output VBL,
  output BW,
  output nBGCLIP,
  output nOBCLIP,
  output nTR,
  output nTG,
  output nTB,
  output CLPO,
  output CLPB,
  output BLACK
);

  wire d_latch_1_q, d_latch_2_q, d_latch_10_q, d_latch_11_q, multiplexer_1_out, multiplexer_2_out,
       multiplexer_3_out, multiplexer_4_out, multiplexer_5_out, multiplexer_6_out, multiplexer_7_out,
       multiplexer_8_out, multiplexer_9_out, multiplexer_10_out, multiplexer_11_out, multiplexer_12_out,
       multiplexer_13_out, multiplexer_14_out, nor_1_out, nor_2_out, nor_3_out, nor_5_out, nor_6_out,
       nor_7_out, nor_8_out, nor_9_out, nor_10_out, nor_14_out, nor_15_out, nor_17_out, nor_18_out,
       nor_19_out, not_1_out, not_2_out, not_3_out, not_4_out, not_5_out;

  not not_1 (not_1_out, PCLK);
  nor nor_1 (nor_1_out, nDBE, nW0);
  nor nor_2 (nor_2_out, nDBE, nW1);
  not not_2 (not_2_out, nor_1_out);
  not not_3 (not_3_out, nor_2_out);
  D_latch d_latch_1 (.EN(not_1_out), .D(nVIS), .Q(d_latch_1_q));  // open: NOT_Q
  D_latch d_latch_2 (.EN(not_1_out), .D(CLIP_B), .Q(d_latch_2_q));  // open: NOT_Q
  D_latch d_latch_3 (.EN(not_1_out), .D(nor_15_out), .Q(CLPO));  // open: NOT_Q
  nor nor_3 (nor_3_out, RC, ~multiplexer_1_out);  // NOR_Gate
  Multiplexer multiplexer_1 (.in0(nor_3_out), .in1(DB2), .out(multiplexer_1_out), .sel(nor_1_out));  // open: en
  D_latch d_latch_4 (.EN(not_2_out), .D(nor_3_out), .Q(I1_32));  // open: NOT_Q
  nor nor_4 (BW, RC, ~multiplexer_2_out);  // NOR_Gate
  Multiplexer multiplexer_2 (.in0(BW), .in1(DB0), .out(multiplexer_2_out), .sel(nor_2_out));  // open: en
  Multiplexer multiplexer_3 (.in0(nor_5_out), .in1(DB3), .out(multiplexer_3_out), .sel(nor_1_out));  // open: en
  D_latch d_latch_5 (.EN(not_2_out), .D(nor_5_out), .NOT_Q(OBSEL));  // open: Q
  Multiplexer multiplexer_4 (.in0(nor_6_out), .in1(DB1), .out(multiplexer_4_out), .sel(nor_2_out));  // open: en
  D_latch d_latch_6 (.EN(not_3_out), .D(nor_6_out), .Q(nBGCLIP));  // open: NOT_Q
  nor nor_5 (nor_5_out, RC, ~multiplexer_3_out);  // NOR_Gate
  nor nor_6 (nor_6_out, RC, ~multiplexer_4_out);  // NOR_Gate
  nor nor_7 (nor_7_out, RC, ~multiplexer_5_out);  // NOR_Gate
  Multiplexer multiplexer_5 (.in0(nor_7_out), .in1(DB4), .out(multiplexer_5_out), .sel(nor_1_out));  // open: en
  D_latch d_latch_7 (.EN(not_2_out), .D(nor_7_out), .NOT_Q(BGSEL));  // open: Q
  nor nor_8 (nor_8_out, RC, ~multiplexer_6_out);  // NOR_Gate
  Multiplexer multiplexer_6 (.in0(nor_8_out), .in1(DB2), .out(multiplexer_6_out), .sel(nor_2_out));  // open: en
  D_latch d_latch_8 (.EN(not_3_out), .D(nor_8_out), .Q(nOBCLIP));  // open: NOT_Q
  nor nor_9 (nor_9_out, RC, ~multiplexer_7_out);  // NOR_Gate
  Multiplexer multiplexer_7 (.in0(nor_9_out), .in1(DB5), .out(multiplexer_7_out), .sel(nor_1_out));  // open: en
  D_latch d_latch_9 (.EN(not_2_out), .D(nor_9_out), .Q(O8_16));  // open: NOT_Q
  nor nor_10 (nor_10_out, RC, ~multiplexer_8_out);  // NOR_Gate
  Multiplexer multiplexer_8 (.in0(nor_10_out), .in1(DB3), .out(multiplexer_8_out), .sel(nor_2_out));  // open: en
  D_latch d_latch_10 (.EN(not_3_out), .D(nor_10_out), .Q(d_latch_10_q));  // open: NOT_Q
  not not_4 (not_4_out, d_latch_10_q);
  nor nor_11 (CLPB, d_latch_2_q, not_4_out, d_latch_1_q);
  nor nor_12 (BLACK, d_latch_10_q, d_latch_11_q);
  nor nor_13 (nSLAVE, RC, ~multiplexer_9_out);  // NOR_Gate
  Multiplexer multiplexer_9 (.in0(nSLAVE), .in1(DB6), .out(multiplexer_9_out), .sel(nor_1_out));  // open: en
  nor nor_14 (nor_14_out, RC, ~multiplexer_10_out);  // NOR_Gate
  Multiplexer multiplexer_10 (.in0(nor_14_out), .in1(DB4), .out(multiplexer_10_out), .sel(nor_2_out));  // open: en
  D_latch d_latch_11 (.EN(not_3_out), .D(nor_14_out), .Q(d_latch_11_q));  // open: NOT_Q
  nor nor_15 (nor_15_out, CLIP_O, d_latch_1_q, not_5_out);
  not not_5 (not_5_out, d_latch_11_q);
  nor nor_16 (VBL, RC, ~multiplexer_11_out);  // NOR_Gate
  Multiplexer multiplexer_11 (.in0(VBL), .in1(DB7), .out(multiplexer_11_out), .sel(nor_1_out));  // open: en
  nor nor_17 (nor_17_out, RC, ~multiplexer_12_out);  // NOR_Gate
  Multiplexer multiplexer_12 (.in0(nor_17_out), .in1(DB5), .out(multiplexer_12_out), .sel(nor_2_out));  // open: en
  D_latch d_latch_12 (.EN(not_3_out), .D(nor_17_out), .NOT_Q(nTR));  // open: Q
  nor nor_18 (nor_18_out, RC, ~multiplexer_13_out);  // NOR_Gate
  Multiplexer multiplexer_13 (.in0(nor_18_out), .in1(DB6), .out(multiplexer_13_out), .sel(nor_2_out));  // open: en
  D_latch d_latch_13 (.EN(not_3_out), .D(nor_18_out), .NOT_Q(nTG));  // open: Q
  not not_6 (nTB, nor_19_out);
  nor nor_19 (nor_19_out, RC, ~multiplexer_14_out);  // NOR_Gate
  Multiplexer multiplexer_14 (.in0(nor_19_out), .in1(DB7), .out(multiplexer_14_out), .sel(nor_2_out));  // open: en

  // Notes on the sheet:
  //   $2000
  //   $2001
endmodule

module MUX (
  input  EXT3_IN,
  input  EXT2_IN,
  input  EXT1_IN,
  input  EXT0_IN,
  input  PCLK,
  input  BGC0,
  input  BGC1,
  input  BGC2,
  input  BGC3,
  input  ZCOL0,
  input  ZCOL1,
  input  ZCOL2,
  input  ZCOL3,
  input  ZPRIO,
  input  THO0,
  input  THO1,
  input  THO2,
  input  THO3,
  input  THO4,
  input  TH_MUX,
  input  SPR0HIT,
  input  LOL,
  input  nVIS,
  input  RESCL,
  input  nDBE,
  input  nR2,
  output EXT0_OUT,
  output EXT1_OUT,
  output EXT2_OUT,
  output EXT3_OUT,
  output PAL0,
  output PAL1,
  output PAL2,
  output PAL3,
  output PAL4,
  output DB6
);

  wire and_1_out, d_latch_1_not_q, d_latch_2_not_q, d_latch_3_not_q, d_latch_4_not_q, d_latch_5_not_q,
       d_latch_6_not_q, d_latch_7_not_q, d_latch_8_not_q, d_latch_9_not_q, d_latch_10_not_q,
       d_latch_11_not_q, d_latch_12_not_q, d_latch_13_not_q, d_latch_14_not_q, d_latch_15_not_q,
       d_latch_16_q, d_latch_17_q, d_latch_18_not_q, d_latch_19_not_q, d_latch_20_not_q, d_latch_21_not_q,
       multiplexer_1_out, multiplexer_2_out, multiplexer_3_out, multiplexer_4_out, multiplexer_5_out,
       multiplexer_6_out, multiplexer_7_out, multiplexer_8_out, multiplexer_9_out, multiplexer_10_out,
       multiplexer_11_out, multiplexer_12_out, multiplexer_13_out, nor_1_out, nor_2_out, nor_3_out,
       nor_4_out, nor_5_out, nor_6_out, nor_7_out, not_1_out, not_2_out, not_3_out, not_4_out, not_9_out,
       or_1_out;

  not not_1 (not_1_out, ZCOL2);
  not not_2 (not_2_out, ZCOL3);
  not not_3 (not_3_out, ZPRIO);
  nor nor_1 (nor_1_out, nDBE, nR2);
  nor nor_2 (nor_2_out, BGC1, BGC0);
  D_latch d_latch_1 (.EN(PCLK), .D(ZCOL0), .NOT_Q(d_latch_1_not_q));  // open: Q
  D_latch d_latch_2 (.EN(PCLK), .D(ZCOL1), .NOT_Q(d_latch_2_not_q));  // open: Q
  D_latch d_latch_3 (.EN(PCLK), .D(not_1_out), .NOT_Q(d_latch_3_not_q));  // open: Q
  D_latch d_latch_4 (.EN(PCLK), .D(not_2_out), .NOT_Q(d_latch_4_not_q));  // open: Q
  D_latch d_latch_5 (.EN(PCLK), .D(not_3_out), .NOT_Q(d_latch_5_not_q));  // open: Q
  D_latch d_latch_6 (.EN(PCLK), .D(THO0), .NOT_Q(d_latch_6_not_q));  // open: Q
  D_latch d_latch_7 (.EN(PCLK), .D(THO1), .NOT_Q(d_latch_7_not_q));  // open: Q
  D_latch d_latch_8 (.EN(PCLK), .D(THO2), .NOT_Q(d_latch_8_not_q));  // open: Q
  D_latch d_latch_9 (.EN(PCLK), .D(THO3), .NOT_Q(d_latch_9_not_q));  // open: Q
  D_latch d_latch_10 (.EN(PCLK), .D(THO4), .NOT_Q(d_latch_10_not_q));  // open: Q
  Multiplexer #(.enable("false")) multiplexer_1 (
    .in0(BGC0), .in1(d_latch_1_not_q), .out(multiplexer_1_out), .sel(nor_6_out));
  Multiplexer #(.enable("false")) multiplexer_2 (
    .in0(BGC1), .in1(d_latch_2_not_q), .out(multiplexer_2_out), .sel(nor_6_out));
  Multiplexer #(.enable("false")) multiplexer_3 (
    .in0(BGC2), .in1(d_latch_3_not_q), .out(multiplexer_3_out), .sel(nor_6_out));
  Multiplexer #(.enable("false")) multiplexer_4 (
    .in0(BGC3), .in1(d_latch_4_not_q), .out(multiplexer_4_out), .sel(nor_6_out));
  not not_4 (not_4_out, nor_2_out);
  not not_5 (EXT0_OUT, multiplexer_1_out);
  not not_6 (EXT1_OUT, multiplexer_2_out);
  not not_7 (EXT2_OUT, multiplexer_3_out);
  not not_8 (EXT3_OUT, multiplexer_4_out);
  or or_1 (or_1_out, d_latch_1_not_q, d_latch_2_not_q);
  nor nor_3 (nor_3_out, nor_2_out, PCLK, SPR0HIT, LOL, nVIS);
  and and_1 (and_1_out, not_4_out, d_latch_5_not_q);
  nor nor_4 (nor_4_out, nor_3_out, nor_5_out);
  nor nor_5 (nor_5_out, nor_4_out, RESCL);
  not not_9 (not_9_out, PCLK);
  nor nor_6 (nor_6_out, and_1_out, or_1_out);
  D_latch d_latch_11 (.EN(not_9_out), .D(EXT0_OUT), .NOT_Q(d_latch_11_not_q));  // open: Q
  D_latch d_latch_12 (.EN(not_9_out), .D(EXT1_OUT), .NOT_Q(d_latch_12_not_q));  // open: Q
  D_latch d_latch_13 (.EN(not_9_out), .D(EXT2_OUT), .NOT_Q(d_latch_13_not_q));  // open: Q
  D_latch d_latch_14 (.EN(not_9_out), .D(EXT3_OUT), .NOT_Q(d_latch_14_not_q));  // open: Q
  D_latch d_latch_15 (.EN(not_9_out), .D(nor_6_out), .NOT_Q(d_latch_15_not_q));  // open: Q
  D_latch d_latch_16 (.EN(not_9_out), .D(not_4_out), .Q(d_latch_16_q));  // open: NOT_Q
  D_latch d_latch_17 (.EN(not_9_out), .D(or_1_out), .Q(d_latch_17_q));  // open: NOT_Q
  nor nor_7 (nor_7_out, d_latch_16_q, d_latch_17_q);
  Multiplexer #(.enable("false")) multiplexer_5 (
    .in0(d_latch_11_not_q), .in1(EXT0_IN), .out(multiplexer_5_out), .sel(nor_7_out));
  Multiplexer #(.enable("false")) multiplexer_6 (
    .in0(d_latch_12_not_q), .in1(EXT1_IN), .out(multiplexer_6_out), .sel(nor_7_out));
  Multiplexer #(.enable("false")) multiplexer_7 (
    .in0(d_latch_13_not_q), .in1(EXT2_IN), .out(multiplexer_7_out), .sel(nor_7_out));
  Multiplexer #(.enable("false")) multiplexer_8 (
    .in0(d_latch_14_not_q), .in1(EXT3_IN), .out(multiplexer_8_out), .sel(nor_7_out));
  D_latch d_latch_18 (.EN(PCLK), .D(multiplexer_5_out), .NOT_Q(d_latch_18_not_q));  // open: Q
  D_latch d_latch_19 (.EN(PCLK), .D(multiplexer_6_out), .NOT_Q(d_latch_19_not_q));  // open: Q
  D_latch d_latch_20 (.EN(PCLK), .D(multiplexer_7_out), .NOT_Q(d_latch_20_not_q));  // open: Q
  D_latch d_latch_21 (.EN(PCLK), .D(multiplexer_8_out), .NOT_Q(d_latch_21_not_q));  // open: Q
  Multiplexer #(.enable("false")) multiplexer_9 (
    .in0(d_latch_18_not_q), .in1(d_latch_6_not_q), .out(multiplexer_9_out), .sel(TH_MUX));
  Multiplexer #(.enable("false")) multiplexer_10 (
    .in0(d_latch_19_not_q), .in1(d_latch_7_not_q), .out(multiplexer_10_out), .sel(TH_MUX));
  Multiplexer #(.enable("false")) multiplexer_11 (
    .in0(d_latch_20_not_q), .in1(d_latch_8_not_q), .out(multiplexer_11_out), .sel(TH_MUX));
  Multiplexer #(.enable("false")) multiplexer_12 (
    .in0(d_latch_21_not_q), .in1(d_latch_9_not_q), .out(multiplexer_12_out), .sel(TH_MUX));
  Multiplexer #(.enable("false")) multiplexer_13 (
    .in0(d_latch_15_not_q), .in1(d_latch_10_not_q), .out(multiplexer_13_out), .sel(TH_MUX));
  Multiplexer multiplexer_14 (.in0(1'b0), .in1(1'b1), .out(DB6), .sel(nor_5_out), .en(nor_1_out));
  D_latch d_latch_22 (.EN(PCLK), .D(multiplexer_13_out), .NOT_Q(PAL4));  // open: Q
  not not_10 (PAL0, multiplexer_9_out);
  not not_11 (PAL1, multiplexer_10_out);
  not not_12 (PAL2, multiplexer_11_out);
  not not_13 (PAL3, multiplexer_12_out);

  // Notes on the sheet:
  //   TH contain directly loaded color
  //   R2'
  //   Sprite/background
  //    strike test
  //   MUX - select one of 4 sources for final color output
  //   OCOL
  //   External/Prev
  //   EXT
  //   Direct/Prev
  //   TRI-STATE
endmodule

module OAM_SUB (
  input  PCLK,
  input  OB0,
  input  OB1,
  input  OB2,
  input  OB3,
  input  OB4,
  input  OB5,
  input  OB6,
  input  OB7,
  input  V0,
  input  V1,
  input  V2,
  input  V3,
  input  V4,
  input  V5,
  input  V6,
  input  V7,
  output OV0,
  output OV1,
  output OV2,
  output OV3,
  output OV4,
  output OV5,
  output OV6,
  output OV7
);

  wire d_latch_1_not_q, d_latch_2_not_q, d_latch_3_not_q, d_latch_4_not_q, d_latch_5_not_q, d_latch_6_not_q,
       d_latch_7_not_q, d_latch_8_not_q, nand_1_out, nand_2_out, nand_3_out, nand_4_out, nand_5_out,
       nand_6_out, nand_7_out, nand_8_out, nor_1_out, nor_2_out, nor_3_out, nor_4_out, nor_5_out, nor_6_out,
       nor_7_out, nor_8_out, nor_9_out, nor_10_out, nor_11_out, nor_12_out, nor_13_out, nor_14_out,
       nor_15_out, nor_16_out, nor_17_out, nor_18_out, nor_19_out, nor_20_out, nor_21_out, nor_22_out,
       nor_23_out, nor_24_out, nor_25_out, nor_26_out, nor_27_out, nor_28_out, nor_29_out, nor_30_out,
       nor_31_out, nor_32_out, nor_33_out, nor_34_out, nor_35_out, nor_36_out, not_1_out, not_2_out,
       not_3_out, not_4_out, not_5_out, not_6_out, not_7_out, not_8_out;

  D_latch d_latch_1 (.EN(PCLK), .D(OB0), .NOT_Q(d_latch_1_not_q));  // open: Q
  D_latch d_latch_2 (.EN(PCLK), .D(OB1), .NOT_Q(d_latch_2_not_q));  // open: Q
  D_latch d_latch_3 (.EN(PCLK), .D(OB2), .NOT_Q(d_latch_3_not_q));  // open: Q
  D_latch d_latch_4 (.EN(PCLK), .D(OB3), .NOT_Q(d_latch_4_not_q));  // open: Q
  D_latch d_latch_5 (.EN(PCLK), .D(OB4), .NOT_Q(d_latch_5_not_q));  // open: Q
  D_latch d_latch_6 (.EN(PCLK), .D(OB5), .NOT_Q(d_latch_6_not_q));  // open: Q
  D_latch d_latch_7 (.EN(PCLK), .D(OB6), .NOT_Q(d_latch_7_not_q));  // open: Q
  D_latch d_latch_8 (.EN(PCLK), .D(OB7), .NOT_Q(d_latch_8_not_q));  // open: Q
  nor nor_1 (nor_1_out, d_latch_1_not_q, V0);
  nand nand_1 (nand_1_out, V0, d_latch_1_not_q);
  nor nor_2 (nor_2_out, d_latch_2_not_q, V1);
  nand nand_2 (nand_2_out, V1, d_latch_2_not_q);
  nor nor_3 (nor_3_out, d_latch_3_not_q, V2);
  nand nand_3 (nand_3_out, V2, d_latch_3_not_q);
  nor nor_4 (nor_4_out, d_latch_4_not_q, V3);
  nand nand_4 (nand_4_out, V3, d_latch_4_not_q);
  nor nor_5 (nor_5_out, d_latch_5_not_q, V4);
  nand nand_5 (nand_5_out, V4, d_latch_5_not_q);
  nor nor_6 (nor_6_out, d_latch_6_not_q, V5);
  nand nand_6 (nand_6_out, V5, d_latch_6_not_q);
  nor nor_7 (nor_7_out, d_latch_7_not_q, V6);
  nand nand_7 (nand_7_out, V6, d_latch_7_not_q);
  nor nor_8 (nor_8_out, d_latch_8_not_q, V7);
  nand nand_8 (nand_8_out, V7, d_latch_8_not_q);
  not not_1 (not_1_out, nand_1_out);
  not not_2 (not_2_out, nand_3_out);
  not not_3 (not_3_out, nand_5_out);
  not not_4 (not_4_out, nand_7_out);
  nor nor_9 (nor_9_out, nor_1_out, not_1_out);
  not not_5 (not_5_out, nand_2_out);
  nor nor_10 (nor_10_out, nor_2_out, nand_1_out);
  nor nor_11 (nor_11_out, nor_2_out, 1'b0, nor_1_out);
  nor nor_12 (nor_12_out, nor_3_out, not_2_out);
  not not_6 (not_6_out, nand_4_out);
  nor nor_13 (nor_13_out, nor_4_out, nand_3_out);
  nor nor_14 (nor_14_out, nor_4_out, nor_30_out, nor_3_out);
  nor nor_15 (nor_15_out, nor_5_out, not_3_out);
  not not_7 (not_7_out, nand_6_out);
  nor nor_16 (nor_16_out, nor_6_out, nand_5_out);
  nor nor_17 (nor_17_out, nor_6_out, nor_32_out, nor_5_out);
  nor nor_18 (nor_18_out, nor_7_out, not_4_out);
  not not_8 (not_8_out, nand_8_out);
  nor nor_19 (nor_19_out, nor_8_out, nand_7_out);
  nor nor_20 (nor_20_out, nor_8_out, nor_34_out, nor_7_out);
  nor nor_21 (nor_21_out, 1'b0, nor_1_out);
  nor nor_22 (nor_22_out, nor_2_out, not_5_out);
  nor nor_23 (nor_23_out, nor_30_out, nor_3_out);
  nor nor_24 (nor_24_out, nor_4_out, not_6_out);
  nor nor_25 (nor_25_out, nor_32_out, nor_5_out);
  nor nor_26 (nor_26_out, nor_6_out, not_7_out);
  nor nor_27 (nor_27_out, nor_34_out, nor_7_out);
  nor nor_28 (nor_28_out, nor_8_out, not_8_out);
  xnor xnor_1 (OV0, nor_9_out, 1'b0);
  nor nor_29 (nor_29_out, nor_21_out, not_1_out);
  xnor xnor_2 (OV1, nor_29_out, nor_22_out);
  nor nor_30 (nor_30_out, not_5_out, nor_10_out, nor_11_out);
  xnor xnor_3 (OV2, nor_12_out, nor_30_out);
  nor nor_31 (nor_31_out, nor_23_out, not_2_out);
  xnor xnor_4 (OV3, nor_31_out, nor_24_out);
  nor nor_32 (nor_32_out, not_6_out, nor_13_out, nor_14_out);
  xnor xnor_5 (OV4, nor_15_out, nor_32_out);
  nor nor_33 (nor_33_out, nor_25_out, not_3_out);
  xnor xnor_6 (OV5, nor_33_out, nor_26_out);
  nor nor_34 (nor_34_out, not_7_out, nor_16_out, nor_17_out);
  xnor xnor_7 (OV6, nor_18_out, nor_34_out);
  nor nor_35 (nor_35_out, nor_27_out, not_4_out);
  xnor xnor_8 (OV7, nor_35_out, nor_28_out);
  nor nor_36 (nor_36_out, not_8_out, nor_19_out, nor_20_out);

  // Notes on the sheet:
  //   S=V-OB
  //   8-BIT SIGNED SUBTRACT
endmodule
module OAM_COUNTER (
  input  POLY,
  input  STEP,
  input  LOAD,
  input  D0,
  input  RES,
  input  D1,
  input  D2,
  input  D3,
  input  D4,
  input  D5,
  input  D6,
  input  D7,
  output out0,
  output out1,
  output out2,
  output out3,
  output out4,
  output out5,
  output out6,
  output out7,
  output COUT
);

  wire and_1_out, and_2_out, and_3_out, and_4_out, and_5_out, and_6_out, and_7_out, and_8_out, and_9_out,
       and_10_out, and_11_out, controlled_buffer_1_out, controlled_buffer_4_out, controlled_buffer_7_out,
       controlled_buffer_10_out, controlled_buffer_13_out, controlled_buffer_16_out,
       controlled_buffer_19_out, controlled_buffer_22_out, d_latch_1_q, d_latch_2_q, d_latch_3_q,
       d_latch_4_q, d_latch_5_q, d_latch_6_q, d_latch_7_q, d_latch_8_q, d_latch_9_not_q, d_latch_10_not_q,
       d_latch_11_not_q, d_latch_12_not_q, d_latch_13_not_q, d_latch_14_not_q, d_latch_15_not_q,
       d_latch_16_not_q, multiplexer_1_out, multiplexer_2_out, multiplexer_3_out, multiplexer_4_out,
       multiplexer_5_out, multiplexer_6_out, multiplexer_7_out, multiplexer_8_out, nand_1_out, nand_2_out,
       nand_3_out, nand_4_out, nand_5_out, nand_6_out, nor_1_out, nor_2_out, nor_3_out, nor_4_out, nor_5_out,
       nor_6_out, nor_7_out, nor_8_out, nor_9_out, nor_10_out, nor_11_out, nor_12_out, nor_13_out,
       nor_14_out, nor_15_out, nor_16_out, nor_17_out, nor_18_out, nor_20_out, nor_21_out, nor_22_out,
       nor_23_out, not_1_out, not_2_out, not_3_out, not_4_out, not_5_out, not_6_out, not_7_out, not_8_out,
       not_9_out, not_10_out, not_11_out, not_12_out, not_13_out, not_14_out, not_15_out, not_16_out,
       or_1_out;

  nor nor_1 (nor_1_out, LOAD, STEP);
  nor nor_2 (nor_2_out, RES, d_latch_9_not_q);
  nor nor_3 (nor_3_out, RES, d_latch_10_not_q);
  nor nor_4 (nor_4_out, RES, d_latch_11_not_q);
  nor nor_5 (nor_5_out, RES, d_latch_12_not_q);
  nor nor_6 (nor_6_out, RES, d_latch_13_not_q);
  nor nor_7 (nor_7_out, RES, d_latch_14_not_q);
  nor nor_8 (nor_8_out, RES, d_latch_15_not_q);
  nor nor_9 (nor_9_out, RES, d_latch_16_not_q);
  Multiplexer #(.enable("false")) multiplexer_1 (
    .in0(d_latch_9_not_q), .in1(nor_2_out), .out(multiplexer_1_out), .sel(1'b1));
  Multiplexer #(.enable("false")) multiplexer_2 (
    .in0(d_latch_10_not_q), .in1(nor_3_out), .out(multiplexer_2_out), .sel(nor_12_out));
  Multiplexer #(.enable("false")) multiplexer_3 (
    .in0(d_latch_11_not_q), .in1(nor_4_out), .out(multiplexer_3_out), .sel(and_1_out));
  Multiplexer #(.enable("false")) multiplexer_4 (
    .in0(d_latch_12_not_q), .in1(nor_5_out), .out(multiplexer_4_out), .sel(and_2_out));
  Multiplexer #(.enable("false")) multiplexer_5 (
    .in0(d_latch_13_not_q), .in1(nor_6_out), .out(multiplexer_5_out), .sel(and_3_out));
  Multiplexer #(.enable("false")) multiplexer_6 (
    .in0(d_latch_14_not_q), .in1(nor_7_out), .out(multiplexer_6_out), .sel(and_4_out));
  Multiplexer #(.enable("false")) multiplexer_7 (
    .in0(d_latch_15_not_q), .in1(nor_8_out), .out(multiplexer_7_out), .sel(and_5_out));
  Multiplexer #(.enable("false")) multiplexer_8 (
    .in0(d_latch_16_not_q), .in1(nor_9_out), .out(multiplexer_8_out), .sel(and_6_out));
  D_latch d_latch_1 (.EN(nor_1_out), .D(multiplexer_1_out), .Q(d_latch_1_q));  // open: NOT_Q
  D_latch d_latch_2 (.EN(nor_1_out), .D(multiplexer_2_out), .Q(d_latch_2_q));  // open: NOT_Q
  D_latch d_latch_3 (.EN(nor_1_out), .D(multiplexer_3_out), .Q(d_latch_3_q));  // open: NOT_Q
  D_latch d_latch_4 (.EN(nor_1_out), .D(multiplexer_4_out), .Q(d_latch_4_q));  // open: NOT_Q
  D_latch d_latch_5 (.EN(nor_1_out), .D(multiplexer_5_out), .Q(d_latch_5_q));  // open: NOT_Q
  D_latch d_latch_6 (.EN(nor_1_out), .D(multiplexer_6_out), .Q(d_latch_6_q));  // open: NOT_Q
  D_latch d_latch_7 (.EN(nor_1_out), .D(multiplexer_7_out), .Q(d_latch_7_q));  // open: NOT_Q
  D_latch d_latch_8 (.EN(nor_1_out), .D(multiplexer_8_out), .Q(d_latch_8_q));  // open: NOT_Q
  nor nor_10 (nor_10_out, d_latch_1_q, POLY);
  not not_1 (not_1_out, 1'b1);
  nor nor_11 (nor_11_out, d_latch_2_q, POLY);
  not not_2 (not_2_out, d_latch_3_q);
  not not_3 (not_3_out, d_latch_4_q);
  not not_4 (not_4_out, d_latch_5_q);
  not not_5 (not_5_out, d_latch_6_q);
  not not_6 (not_6_out, d_latch_7_q);
  not not_7 (not_7_out, d_latch_8_q);
  assign controlled_buffer_1_out = LOAD ? D0 : 1'bz;  // Controlled_Buffer controlled_buffer_1
  assign controlled_buffer_1_out = STEP ? nor_10_out : 1'bz;  // Controlled_Buffer controlled_buffer_2
  assign controlled_buffer_1_out = nor_1_out ? nor_2_out : 1'bz;  // Controlled_Buffer controlled_buffer_3
  assign controlled_buffer_4_out = LOAD ? D1 : 1'bz;  // Controlled_Buffer controlled_buffer_4
  assign controlled_buffer_4_out = STEP ? nor_11_out : 1'bz;  // Controlled_Buffer controlled_buffer_5
  assign controlled_buffer_4_out = nor_1_out ? nor_3_out : 1'bz;  // Controlled_Buffer controlled_buffer_6
  assign controlled_buffer_7_out = LOAD ? D2 : 1'bz;  // Controlled_Buffer controlled_buffer_7
  assign controlled_buffer_7_out = STEP ? not_2_out : 1'bz;  // Controlled_Buffer controlled_buffer_8
  assign controlled_buffer_7_out = nor_1_out ? nor_4_out : 1'bz;  // Controlled_Buffer controlled_buffer_9
  assign controlled_buffer_10_out = LOAD ? D3 : 1'bz;  // Controlled_Buffer controlled_buffer_10
  assign controlled_buffer_10_out = STEP ? not_3_out : 1'bz;  // Controlled_Buffer controlled_buffer_11
  assign controlled_buffer_10_out = nor_1_out ? nor_5_out : 1'bz;  // Controlled_Buffer controlled_buffer_12
  assign controlled_buffer_13_out = LOAD ? D4 : 1'bz;  // Controlled_Buffer controlled_buffer_13
  assign controlled_buffer_13_out = STEP ? not_4_out : 1'bz;  // Controlled_Buffer controlled_buffer_14
  assign controlled_buffer_13_out = nor_1_out ? nor_6_out : 1'bz;  // Controlled_Buffer controlled_buffer_15
  assign controlled_buffer_16_out = LOAD ? D5 : 1'bz;  // Controlled_Buffer controlled_buffer_16
  assign controlled_buffer_16_out = STEP ? not_5_out : 1'bz;  // Controlled_Buffer controlled_buffer_17
  assign controlled_buffer_16_out = nor_1_out ? nor_7_out : 1'bz;  // Controlled_Buffer controlled_buffer_18
  assign controlled_buffer_19_out = LOAD ? D6 : 1'bz;  // Controlled_Buffer controlled_buffer_19
  assign controlled_buffer_19_out = STEP ? not_6_out : 1'bz;  // Controlled_Buffer controlled_buffer_20
  assign controlled_buffer_19_out = nor_1_out ? nor_8_out : 1'bz;  // Controlled_Buffer controlled_buffer_21
  assign controlled_buffer_22_out = LOAD ? D7 : 1'bz;  // Controlled_Buffer controlled_buffer_22
  assign controlled_buffer_22_out = STEP ? not_7_out : 1'bz;  // Controlled_Buffer controlled_buffer_23
  assign controlled_buffer_22_out = nor_1_out ? nor_9_out : 1'bz;  // Controlled_Buffer controlled_buffer_24
  D_latch d_latch_9 (.EN(1'b1), .D(controlled_buffer_1_out), .Q(out0), .NOT_Q(d_latch_9_not_q));
  D_latch d_latch_10 (.EN(1'b1), .D(controlled_buffer_4_out), .Q(out1), .NOT_Q(d_latch_10_not_q));
  D_latch d_latch_11 (.EN(1'b1), .D(controlled_buffer_7_out), .Q(out2), .NOT_Q(d_latch_11_not_q));
  D_latch d_latch_12 (.EN(1'b1), .D(controlled_buffer_10_out), .Q(out3), .NOT_Q(d_latch_12_not_q));
  D_latch d_latch_13 (.EN(1'b1), .D(controlled_buffer_13_out), .Q(out4), .NOT_Q(d_latch_13_not_q));
  D_latch d_latch_14 (.EN(1'b1), .D(controlled_buffer_16_out), .Q(out5), .NOT_Q(d_latch_14_not_q));
  D_latch d_latch_15 (.EN(1'b1), .D(controlled_buffer_19_out), .Q(out6), .NOT_Q(d_latch_15_not_q));
  D_latch d_latch_16 (.EN(1'b1), .D(controlled_buffer_22_out), .Q(out7), .NOT_Q(d_latch_16_not_q));
  not not_8 (not_8_out, POLY);
  nor nor_12 (nor_12_out, not_1_out, d_latch_9_not_q);
  not not_9 (not_9_out, nor_12_out);
  nor nor_13 (nor_13_out, not_9_out, d_latch_10_not_q);
  and and_1 (and_1_out, nor_13_out, nand_1_out);
  not not_10 (not_10_out, and_1_out);
  nor nor_14 (nor_14_out, not_10_out, d_latch_11_not_q);
  and and_2 (and_2_out, nor_14_out, and_7_out);
  not not_11 (not_11_out, and_2_out);
  nor nor_15 (nor_15_out, not_11_out, d_latch_12_not_q);
  and and_3 (and_3_out, nor_15_out, and_8_out);
  not not_12 (not_12_out, and_3_out);
  nor nor_16 (nor_16_out, not_12_out, d_latch_13_not_q);
  and and_4 (and_4_out, nor_16_out, and_9_out);
  not not_13 (not_13_out, and_4_out);
  nor nor_17 (nor_17_out, not_13_out, d_latch_14_not_q);
  and and_5 (and_5_out, nor_17_out, and_10_out);
  not not_14 (not_14_out, and_5_out);
  nor nor_18 (nor_18_out, not_14_out, d_latch_15_not_q);
  and and_6 (and_6_out, nor_18_out, and_11_out);
  not not_15 (not_15_out, and_6_out);
  nor nor_19 (COUT, not_15_out, d_latch_16_not_q);
  Pull_Resistor pull_resistor_1 (.node(not_8_out));
  or or_1 (or_1_out, d_latch_9_not_q, d_latch_10_not_q);
  nand nand_1 (nand_1_out, not_8_out, or_1_out);
  nand nand_2 (nand_2_out, not_8_out, or_1_out);
  not not_16 (not_16_out, d_latch_11_not_q);
  nand nand_3 (nand_3_out, not_8_out, or_1_out);
  nor nor_20 (nor_20_out, d_latch_11_not_q, d_latch_12_not_q);
  nand nand_4 (nand_4_out, not_8_out, or_1_out);
  nor nor_21 (nor_21_out, d_latch_11_not_q, d_latch_12_not_q, d_latch_13_not_q);
  nand nand_5 (nand_5_out, not_8_out, or_1_out);
  nor nor_22 (nor_22_out, d_latch_11_not_q, d_latch_12_not_q, d_latch_13_not_q, d_latch_14_not_q);
  nand nand_6 (nand_6_out, or_1_out, not_8_out);
  nor nor_23 (nor_23_out, d_latch_11_not_q, d_latch_12_not_q, d_latch_13_not_q, d_latch_14_not_q, d_latch_15_not_q);
  and and_7 (and_7_out, nand_2_out, not_16_out);
  and and_8 (and_8_out, nand_3_out, nor_20_out);
  and and_9 (and_9_out, nand_4_out, nor_21_out);
  and and_10 (and_10_out, nand_5_out, nor_22_out);
  and and_11 (and_11_out, nand_6_out, nor_23_out);

  // Notes on the sheet:
  //   carry_out
  //   carry_out
  //   carry_out
  //   carry_out
  //   carry_out
  //   carry_out
  //   carry_out
  //   carry_out
endmodule

module OAM_TEMP_COUNTER (
  input  LOAD,
  input  STEP,
  input  D0,
  input  RES
);

  wire controlled_buffer_1_out, d_latch_1_not_q, d_latch_2_not_q, d_latch_2_q, multiplexer_1_out, nor_1_out,
       nor_2_out, nor_3_out, not_1_out;

  nor nor_1 (nor_1_out, STEP, LOAD);
  nor nor_2 (nor_2_out, RES, d_latch_2_not_q);
  Multiplexer #(.enable("false")) multiplexer_1 (
    .in0(d_latch_2_not_q), .in1(nor_2_out), .out(multiplexer_1_out), .sel(1'b1));
  assign controlled_buffer_1_out = nor_1_out ? nor_2_out : 1'bz;  // Controlled_Buffer controlled_buffer_1
  D_latch d_latch_1 (.EN(nor_1_out), .D(multiplexer_1_out), .NOT_Q(d_latch_1_not_q));  // open: Q
  not not_1 (not_1_out, 1'b1);
  assign controlled_buffer_1_out = LOAD ? D0 : 1'bz;  // Controlled_Buffer controlled_buffer_2
  assign controlled_buffer_1_out = STEP ? d_latch_1_not_q : 1'bz;  // Controlled_Buffer controlled_buffer_3
  D_latch d_latch_2 (.EN(1'b1), .D(controlled_buffer_1_out), .Q(d_latch_2_q), .NOT_Q(d_latch_2_not_q));
  nor nor_3 (nor_3_out, not_1_out, d_latch_2_not_q);

  // Notes on the sheet:
  //   carry_out
endmodule

// OAM CONTROL
module OAM_CONTROL (
  input  PCLK,
  input  OFETCH,
  input  BLNK,
  input  nVIS,
  input  H0_prime_prime,
  input  I_OAM2,
  input  OMFG,
  input  nDBE,
  input  nW3,
  input  PAR_O,
  input  DB0,
  input  DB1,
  input  DB2,
  input  DB3,
  input  DB4,
  input  DB5,
  input  DB6,
  input  DB7,
  input  EVAL,
  input  H2_prime,
  input  H0_prime,
  input  RESCL,
  input  nR2,
  output nOAM0,
  output nOAM1,
  output nOAM2,
  output nOAM3,
  output nOAM4,
  output nOAM5,
  output nOAM6,
  output nOAM7,
  output nOAM8,
  output WTF,
  output MILF,
  output DB5_2
);

  wire _14_out, _27_out, and_1_out, d_latch_1_not_q, d_latch_2_q, d_latch_3_not_q, d_latch_4_q, d_latch_5_q,
       d_latch_6_q, d_latch_7_q, d_latch_8_q, d_latch_9_q, d_latch_10_q, multiplexer_1_out,
       multiplexer_2_out, multiplexer_3_out, multiplexer_4_out, multiplexer_5_out, nand_1_out, nand_2_out,
       nand_3_out, nand_4_out, nor_1_out, nor_2_out, nor_3_out, nor_4_out, nor_5_out, nor_6_out, nor_7_out,
       nor_8_out, nor_9_out, nor_10_out, nor_11_out, nor_12_out, nor_13_out, nor_15_out, nor_16_out,
       not_2_out, not_3_out, not_4_out, not_5_out, not_6_out, not_7_out, not_8_out, nPCLK,
       oam_counter_1_cout, oam_counter_1_out0, oam_counter_1_out1, oam_counter_1_out2, oam_counter_1_out3,
       oam_counter_1_out4, oam_counter_1_out5, oam_counter_1_out6, oam_counter_1_out7,
       oam_second_counter_1_carry_out, oam_second_counter_1_nq0, oam_second_counter_1_nq1,
       oam_second_counter_1_nq2, oam_second_counter_1_nq3, oam_second_counter_1_nq4, or_1_out, or_2_out;

  not not_1 (nPCLK, PCLK);
  not not_2 (not_2_out, H2_prime);
  not not_3 (not_3_out, OMFG);
  not not_4 (not_4_out, BLNK);
  nor nor_1 (nor_1_out, nVIS, I_OAM2);
  nor nor_2 (nor_2_out, BLNK, not_5_out);
  not not_5 (not_5_out, OMFG);
  nor nor_3 (nor_3_out, nDBE, nW3);
  nand nand_1 (nand_1_out, EVAL, nor_16_out);
  and and_1 (and_1_out, PAR_O, not_2_out);
  D_latch d_latch_1 (.EN(nPCLK), .D(not_3_out), .NOT_Q(d_latch_1_not_q));  // open: Q
  D_latch d_latch_2 (.EN(nPCLK), .D(I_OAM2), .Q(d_latch_2_q));  // open: NOT_Q
  nor nor_4 (nor_4_out, nR2, nDBE);
  not not_6 (not_6_out, nor_4_out);
  D_latch d_latch_3 (.EN(nPCLK), .D(OFETCH), .NOT_Q(d_latch_3_not_q));  // open: Q
  or or_1 (or_1_out, nVIS, H0_prime_prime);
  nand nand_2 (nand_2_out, H0_prime_prime, nor_1_out);
  D_latch d_latch_4 (.EN(nPCLK), .D(EVAL), .Q(d_latch_4_q));  // open: NOT_Q
  D_latch d_latch_5 (.EN(nPCLK), .D(nand_1_out), .Q(d_latch_5_q));  // open: NOT_Q
  nor nor_5 (nor_5_out, and_1_out, nor_10_out);
  nor nor_6 (nor_6_out, d_latch_1_not_q, d_latch_2_q);
  nor nor_7 (nor_7_out, nPCLK, d_latch_3_not_q);
  nand nand_3 (nand_3_out, not_4_out, or_1_out);
  nor nor_8 (nor_8_out, nPCLK, d_latch_4_q);
  nor nor_9 (nor_9_out, nPCLK, d_latch_5_q, nor_5_out);
  nor nor_10 (nor_10_out, nor_6_out, H0_prime);
  not not_7 (not_7_out, nor_7_out);
  D_latch d_latch_6 (.EN(nPCLK), .D(nand_2_out), .Q(d_latch_6_q));  // open: NOT_Q
  or or_2 (or_2_out, nPCLK, d_latch_6_q);
  nand nand_4 (nand_4_out, or_2_out, not_7_out);
  OAM_COUNTER oam_counter_1 (
    .POLY(nor_2_out), .LOAD(nor_3_out), .STEP(nand_4_out), .RES(PAR_O), .D0(DB0), .D1(DB1), .D2(DB2),
    .D3(DB3), .D4(DB4), .D5(DB5), .D6(DB6), .D7(DB7), .out0(oam_counter_1_out0), .out1(oam_counter_1_out1),
    .out2(oam_counter_1_out2), .out3(oam_counter_1_out3), .out4(oam_counter_1_out4),
    .out5(oam_counter_1_out5), .out6(oam_counter_1_out6), .out7(oam_counter_1_out7), .COUT(oam_counter_1_cout));
  OAM_SECOND_COUNTER oam_second_counter_1 (
    .OSTEP(nor_9_out), .ORES(nor_8_out), .nPCLK(nPCLK), .nQ0(oam_second_counter_1_nq0),
    .nQ1(oam_second_counter_1_nq1), .nQ3(oam_second_counter_1_nq3), .nQ4(oam_second_counter_1_nq4),
    .CARRY_OUT(oam_second_counter_1_carry_out), .nQ2(oam_second_counter_1_nq2));
  D_latch d_latch_7 (.EN(nPCLK), .D(nor_16_out), .Q(d_latch_7_q));  // open: NOT_Q
  D_latch d_latch_8 (.EN(nPCLK), .D(OMFG), .Q(d_latch_8_q));  // open: NOT_Q
  nor nor_11 (nor_11_out, nPCLK, d_latch_7_q, d_latch_8_q, H0_prime);
  nor nor_12 (nor_12_out, nor_11_out, nor_13_out);
  nor nor_13 (nor_13_out, nor_12_out, RESCL);
  D_latch d_latch_9 (.EN(nPCLK), .D(oam_counter_1_cout), .Q(d_latch_9_q));  // open: NOT_Q
  D_latch d_latch_10 (.EN(nPCLK), .D(oam_second_counter_1_carry_out), .Q(d_latch_10_q));  // open: NOT_Q
  Multiplexer #(.enable("false")) multiplexer_1 (
    .in0(oam_second_counter_1_nq0), .in1(oam_counter_1_out0), .out(multiplexer_1_out), .sel(nand_3_out));
  Multiplexer #(.enable("false")) multiplexer_2 (
    .in0(oam_second_counter_1_nq1), .in1(oam_counter_1_out1), .out(multiplexer_2_out), .sel(nand_3_out));
  Multiplexer #(.enable("false")) multiplexer_3 (
    .in0(oam_second_counter_1_nq2), .in1(oam_counter_1_out2), .out(multiplexer_3_out), .sel(nand_3_out));
  Multiplexer #(.enable("false")) multiplexer_4 (
    .in0(oam_second_counter_1_nq3), .in1(oam_counter_1_out3), .out(multiplexer_4_out), .sel(nand_3_out));
  Multiplexer #(.enable("false")) multiplexer_5 (
    .in0(oam_second_counter_1_nq4), .in1(oam_counter_1_out4), .out(multiplexer_5_out), .sel(nand_3_out));
  and _27 (_27_out, nand_4_out, d_latch_9_q);
  and _14 (_14_out, d_latch_10_q, nor_9_out);
  not not_8 (not_8_out, not_6_out);
  not not_9 (nOAM0, multiplexer_1_out);
  not not_10 (nOAM1, multiplexer_2_out);
  not not_11 (nOAM2, multiplexer_3_out);
  not not_12 (nOAM3, multiplexer_4_out);
  not not_13 (nOAM4, multiplexer_5_out);
  not not_14 (nOAM5, oam_counter_1_out5);
  not not_15 (nOAM6, oam_counter_1_out6);
  not not_16 (nOAM7, oam_counter_1_out7);
  not not_17 (nOAM8, nand_3_out);
  nor nor_14 (WTF, I_OAM2, nor_15_out);
  nor nor_15 (nor_15_out, WTF, _27_out, nor_11_out);
  nor nor_16 (nor_16_out, _14_out, MILF);
  nor nor_17 (MILF, nor_16_out, nor_8_out);
  Multiplexer multiplexer_6 (.in0(1'b0), .in1(1'b1), .out(DB5_2), .sel(nor_13_out), .en(not_8_out));

  // Notes on the sheet:
  //   1
  //   6
  //   9
  //   8
  //   25
  //   10
  //   17
  //   20
  //   W3'
  //   4
  //   3
  //   4
  //   1
  //   2
  //   10
  //   18
  //   21
  //   4
  //   2
  //   /R2'
  //   23
  //   24
  //   18
  //   8
  //   ORES
  //   7
  //   5
  //   3
  //   22
  //   22
  //   5
  //   6
  //   OMV
  //   OMV
  //   TMV
  //   13
  //   9
  //   7
  //   Sprite overflow flag
  //   3
  //   OMV'
  //   TMV'
  //   1
  //   2
  //   WTF
  //   ASAP
  //   MILF
  //   TRI-STATE
endmodule

module OAM (
  input  PCLK,
  input  nOAM0,
  input  nOAM1,
  input  nOAM2,
  input  nOAM3,
  input  nOAM4,
  input  nOAM5,
  input  nOAM6,
  input  nOAM7,
  input  OAM8,
  input  OB0_OAM,
  input  OB1_OAM,
  input  OB2_OAM,
  input  OB3_OAM,
  input  OB4_OAM,
  input  OB5_OAM,
  input  OB6_OAM,
  input  OB7_OAM,
  output OAM_OB0,
  output OAM_OB1,
  output OAM_OB2,
  output OAM_OB3,
  output OAM_OB4,
  output OAM_OB5,
  output OAM_OB6,
  output OAM_OB7
);

  wire nor_1_out, nor_2_out, nor_3_out, nor_4_out, nor_5_out, nor_6_out, nor_7_out, nor_8_out, nor_9_out,
       nor_10_out, nor_11_out, nor_12_out, nor_13_out, nor_14_out, nor_15_out, nor_16_out, nor_17_out,
       nor_18_out, nor_19_out, nor_20_out, nor_21_out, nor_22_out, nor_23_out, nor_24_out, nor_25_out,
       nor_26_out, nor_27_out, nor_28_out, nor_29_out, nor_30_out, nor_31_out, nor_32_out, nor_33_out,
       nor_34_out, nor_35_out, nor_36_out, nor_37_out, nor_38_out, nor_39_out, nor_40_out, not_1_out,
       not_2_out, not_3_out, not_4_out, not_5_out, not_6_out, not_7_out, not_8_out;

  not not_1 (not_1_out, nOAM0);
  not not_2 (not_2_out, nOAM1);
  not not_3 (not_3_out, nOAM2);
  not not_4 (not_4_out, nOAM5);
  not not_5 (not_5_out, nOAM6);
  not not_6 (not_6_out, nOAM7);
  not not_7 (not_7_out, nOAM3);
  not not_8 (not_8_out, nOAM4);
  nor nor_1 (nor_1_out, nOAM3, nOAM4, nOAM5, nOAM6, nOAM7);
  nor nor_2 (nor_2_out, not_1_out, not_2_out, not_3_out, OAM8);
  nor nor_3 (nor_3_out, nOAM3, nOAM4, nOAM5, nOAM6, not_6_out);
  nor nor_4 (nor_4_out, nOAM0, not_2_out, not_3_out, OAM8);
  nor nor_5 (nor_5_out, nOAM3, nOAM4, nOAM5, not_5_out, nOAM7);
  nor nor_6 (nor_6_out, not_1_out, nOAM1, not_3_out, OAM8);
  nor nor_7 (nor_7_out, nOAM3, nOAM4, nOAM5, not_5_out, not_6_out);
  nor nor_8 (nor_8_out, nOAM0, nOAM1, not_3_out, OAM8);
  nor nor_9 (nor_9_out, nOAM3, nOAM4, not_4_out, nOAM6, nOAM7);
  nor nor_10 (nor_10_out, not_1_out, not_2_out, nOAM2, OAM8);
  nor nor_11 (nor_11_out, nOAM3, nOAM4, not_4_out, nOAM6, not_6_out);
  nor nor_12 (nor_12_out, nOAM0, not_2_out, nOAM2, OAM8);
  nor nor_13 (nor_13_out, nOAM3, nOAM4, not_4_out, not_5_out, nOAM7);
  nor nor_14 (nor_14_out, not_1_out, nOAM1, nOAM2, OAM8);
  nor nor_15 (nor_15_out, nOAM0, nOAM1, nOAM2, OAM8);
  nor nor_16 (nor_16_out, nOAM3, nOAM4, not_4_out, not_5_out, not_6_out);
  nor nor_17 (nor_17_out, nOAM3, not_8_out, nOAM5, nOAM6, nOAM7);
  nor nor_18 (nor_18_out, nOAM3, not_8_out, nOAM5, nOAM6, not_6_out);
  nor nor_19 (nor_19_out, nOAM3, not_8_out, nOAM5, not_5_out, nOAM7);
  nor nor_20 (nor_20_out, nOAM3, not_8_out, nOAM5, not_5_out, not_6_out);
  OAM_BIG_ROW oam_big_row_1 (
    .PCLK(PCLK), .in_2(nor_4_out), .in_3(nor_8_out), .in_4(nor_12_out), .in_5(nor_15_out), .in_6(nor_2_out),
    .in_7(nor_6_out), .in_8(nor_10_out), .in_9(nor_14_out), .in_10(OAM8), .in_43(OB0_OAM), .out_44(OAM_OB0),
    .in_11(nor_1_out), .in_12(nor_3_out), .in_13(nor_5_out), .in_14(nor_7_out), .in_15(nor_9_out),
    .in_16(nor_11_out), .in_17(nor_13_out), .in_18(nor_16_out), .in_19(nor_17_out), .in_20(nor_18_out),
    .in_21(nor_19_out), .in_22(nor_20_out), .in_23(nor_21_out), .in_24(nor_22_out), .in_25(nor_23_out),
    .in_26(nor_24_out), .in_27(nor_25_out), .in_28(nor_26_out), .in_29(nor_27_out), .in_30(nor_28_out),
    .in_31(nor_29_out), .in_32(nor_30_out), .in_33(nor_31_out), .in_34(nor_32_out), .in_35(nor_33_out),
    .in_36(nor_34_out), .in_37(nor_35_out), .in_38(nor_36_out), .in_39(nor_37_out), .in_40(nor_38_out),
    .in_41(nor_39_out), .in_42(nor_40_out));
  OAM_BIG_ROW oam_big_row_2 (
    .PCLK(PCLK), .in_2(nor_4_out), .in_3(nor_8_out), .in_4(nor_12_out), .in_5(nor_15_out), .in_6(nor_2_out),
    .in_7(nor_6_out), .in_8(nor_10_out), .in_9(nor_14_out), .in_10(OAM8), .in_43(OB1_OAM), .out_44(OAM_OB1),
    .in_11(nor_1_out), .in_12(nor_3_out), .in_13(nor_5_out), .in_14(nor_7_out), .in_15(nor_9_out),
    .in_16(nor_11_out), .in_17(nor_13_out), .in_18(nor_16_out), .in_19(nor_17_out), .in_20(nor_18_out),
    .in_21(nor_19_out), .in_22(nor_20_out), .in_23(nor_21_out), .in_24(nor_22_out), .in_25(nor_23_out),
    .in_26(nor_24_out), .in_27(nor_25_out), .in_28(nor_26_out), .in_29(nor_27_out), .in_30(nor_28_out),
    .in_31(nor_29_out), .in_32(nor_30_out), .in_33(nor_31_out), .in_34(nor_32_out), .in_35(nor_33_out),
    .in_36(nor_34_out), .in_37(nor_35_out), .in_38(nor_36_out), .in_39(nor_37_out), .in_40(nor_38_out),
    .in_41(nor_39_out), .in_42(nor_40_out));
  OAM_BIG_ROW oam_big_row_3 (
    .PCLK(PCLK), .in_2(nor_4_out), .in_3(nor_8_out), .in_4(nor_12_out), .in_5(nor_15_out), .in_6(nor_2_out),
    .in_7(nor_6_out), .in_8(nor_10_out), .in_9(nor_14_out), .in_10(OAM8), .in_43(OB2_OAM), .out_44(OAM_OB2),
    .in_11(nor_1_out), .in_12(nor_3_out), .in_13(nor_5_out), .in_14(nor_7_out), .in_15(nor_9_out),
    .in_16(nor_11_out), .in_17(nor_13_out), .in_18(nor_16_out), .in_19(nor_17_out), .in_20(nor_18_out),
    .in_21(nor_19_out), .in_22(nor_20_out), .in_23(nor_21_out), .in_24(nor_22_out), .in_25(nor_23_out),
    .in_26(nor_24_out), .in_27(nor_25_out), .in_28(nor_26_out), .in_29(nor_27_out), .in_30(nor_28_out),
    .in_31(nor_29_out), .in_32(nor_30_out), .in_33(nor_31_out), .in_34(nor_32_out), .in_35(nor_33_out),
    .in_36(nor_34_out), .in_37(nor_35_out), .in_38(nor_36_out), .in_39(nor_37_out), .in_40(nor_38_out),
    .in_41(nor_39_out), .in_42(nor_40_out));
  OAM_SMALL_ROW oam_small_row_1 (
    .PCLK(PCLK), .in_2(nor_4_out), .in_3(nor_8_out), .in_4(nor_15_out), .in_5(nor_2_out), .in_6(nor_10_out),
    .in_7(nor_12_out), .in_8(OAM8), .in_41(OB3_OAM), .out_42(OAM_OB3), .in_9(nor_1_out), .in_10(nor_3_out),
    .in_11(nor_5_out), .in_12(nor_7_out), .in_13(nor_9_out), .in_14(nor_11_out), .in_15(nor_13_out),
    .in_16(nor_16_out), .in_17(nor_17_out), .in_18(nor_18_out), .in_19(nor_19_out), .in_20(nor_20_out),
    .in_21(nor_21_out), .in_22(nor_22_out), .in_23(nor_23_out), .in_24(nor_24_out), .in_25(nor_25_out),
    .in_26(nor_26_out), .in_27(nor_27_out), .in_28(nor_28_out), .in_29(nor_29_out), .in_30(nor_30_out),
    .in_31(nor_31_out), .in_32(nor_32_out), .in_33(nor_33_out), .in_34(nor_34_out), .in_35(nor_35_out),
    .in_36(nor_36_out), .in_37(nor_37_out), .in_38(nor_38_out), .in_39(nor_39_out), .in_40(nor_40_out));
  OAM_SMALL_ROW oam_small_row_2 (
    .PCLK(PCLK), .in_2(nor_4_out), .in_3(nor_8_out), .in_4(nor_15_out), .in_5(nor_2_out), .in_6(nor_10_out),
    .in_7(nor_12_out), .in_8(OAM8), .in_41(OB4_OAM), .out_42(OAM_OB4), .in_9(nor_1_out), .in_10(nor_3_out),
    .in_11(nor_5_out), .in_12(nor_7_out), .in_13(nor_9_out), .in_14(nor_11_out), .in_15(nor_13_out),
    .in_16(nor_16_out), .in_17(nor_17_out), .in_18(nor_18_out), .in_19(nor_19_out), .in_20(nor_20_out),
    .in_21(nor_21_out), .in_22(nor_22_out), .in_23(nor_23_out), .in_24(nor_24_out), .in_25(nor_25_out),
    .in_26(nor_26_out), .in_27(nor_27_out), .in_28(nor_28_out), .in_29(nor_29_out), .in_30(nor_30_out),
    .in_31(nor_31_out), .in_32(nor_32_out), .in_33(nor_33_out), .in_34(nor_34_out), .in_35(nor_35_out),
    .in_36(nor_36_out), .in_37(nor_37_out), .in_38(nor_38_out), .in_39(nor_39_out), .in_40(nor_40_out));
  OAM_SMALL_ROW oam_small_row_3 (
    .PCLK(PCLK), .in_2(nor_4_out), .in_3(nor_8_out), .in_4(nor_15_out), .in_5(nor_2_out), .in_6(nor_10_out),
    .in_7(nor_12_out), .in_8(OAM8), .in_41(OB5_OAM), .out_42(OAM_OB5), .in_9(nor_1_out), .in_10(nor_3_out),
    .in_11(nor_5_out), .in_12(nor_7_out), .in_13(nor_9_out), .in_14(nor_11_out), .in_15(nor_13_out),
    .in_16(nor_16_out), .in_17(nor_17_out), .in_18(nor_18_out), .in_19(nor_19_out), .in_20(nor_20_out),
    .in_21(nor_21_out), .in_22(nor_22_out), .in_23(nor_23_out), .in_24(nor_24_out), .in_25(nor_25_out),
    .in_26(nor_26_out), .in_27(nor_27_out), .in_28(nor_28_out), .in_29(nor_29_out), .in_30(nor_30_out),
    .in_31(nor_31_out), .in_32(nor_32_out), .in_33(nor_33_out), .in_34(nor_34_out), .in_35(nor_35_out),
    .in_36(nor_36_out), .in_37(nor_37_out), .in_38(nor_38_out), .in_39(nor_39_out), .in_40(nor_40_out));
  OAM_BIG_ROW oam_big_row_4 (
    .PCLK(PCLK), .in_2(nor_4_out), .in_3(nor_8_out), .in_4(nor_12_out), .in_5(nor_15_out), .in_6(nor_2_out),
    .in_7(nor_6_out), .in_8(nor_10_out), .in_9(nor_14_out), .in_10(OAM8), .in_43(OB6_OAM), .out_44(OAM_OB6),
    .in_11(nor_1_out), .in_12(nor_3_out), .in_13(nor_5_out), .in_14(nor_7_out), .in_15(nor_9_out),
    .in_16(nor_11_out), .in_17(nor_13_out), .in_18(nor_16_out), .in_19(nor_17_out), .in_20(nor_18_out),
    .in_21(nor_19_out), .in_22(nor_20_out), .in_23(nor_21_out), .in_24(nor_22_out), .in_25(nor_23_out),
    .in_26(nor_24_out), .in_27(nor_25_out), .in_28(nor_26_out), .in_29(nor_27_out), .in_30(nor_28_out),
    .in_31(nor_29_out), .in_32(nor_30_out), .in_33(nor_31_out), .in_34(nor_32_out), .in_35(nor_33_out),
    .in_36(nor_34_out), .in_37(nor_35_out), .in_38(nor_36_out), .in_39(nor_37_out), .in_40(nor_38_out),
    .in_41(nor_39_out), .in_42(nor_40_out));
  OAM_BIG_ROW oam_big_row_5 (
    .PCLK(PCLK), .in_2(nor_4_out), .in_3(nor_8_out), .in_4(nor_12_out), .in_5(nor_15_out), .in_6(nor_2_out),
    .in_7(nor_6_out), .in_8(nor_10_out), .in_9(nor_14_out), .in_10(OAM8), .in_43(OB7_OAM), .out_44(OAM_OB7),
    .in_11(nor_1_out), .in_12(nor_3_out), .in_13(nor_5_out), .in_14(nor_7_out), .in_15(nor_9_out),
    .in_16(nor_11_out), .in_17(nor_13_out), .in_18(nor_16_out), .in_19(nor_17_out), .in_20(nor_18_out),
    .in_21(nor_19_out), .in_22(nor_20_out), .in_23(nor_21_out), .in_24(nor_22_out), .in_25(nor_23_out),
    .in_26(nor_24_out), .in_27(nor_25_out), .in_28(nor_26_out), .in_29(nor_27_out), .in_30(nor_28_out),
    .in_31(nor_29_out), .in_32(nor_30_out), .in_33(nor_31_out), .in_34(nor_32_out), .in_35(nor_33_out),
    .in_36(nor_34_out), .in_37(nor_35_out), .in_38(nor_36_out), .in_39(nor_37_out), .in_40(nor_38_out),
    .in_41(nor_39_out), .in_42(nor_40_out));
  nor nor_21 (nor_21_out, nOAM3, not_8_out, not_4_out, nOAM6, nOAM7);
  nor nor_22 (nor_22_out, nOAM3, not_8_out, not_4_out, nOAM6, not_6_out);
  nor nor_23 (nor_23_out, nOAM3, not_8_out, not_4_out, not_5_out, nOAM7);
  nor nor_24 (nor_24_out, nOAM3, not_8_out, not_4_out, not_5_out, not_6_out);
  nor nor_25 (nor_25_out, not_7_out, nOAM4, nOAM5, nOAM6, nOAM7);
  nor nor_26 (nor_26_out, not_7_out, nOAM4, nOAM5, nOAM6, not_6_out);
  nor nor_27 (nor_27_out, not_7_out, nOAM4, nOAM5, not_5_out, nOAM7);
  nor nor_28 (nor_28_out, not_7_out, nOAM4, nOAM5, not_5_out, not_6_out);
  nor nor_29 (nor_29_out, not_7_out, nOAM4, not_4_out, nOAM6, nOAM7);
  nor nor_30 (nor_30_out, not_7_out, nOAM4, not_4_out, nOAM6, not_6_out);
  nor nor_31 (nor_31_out, not_7_out, nOAM4, not_4_out, not_5_out, nOAM7);
  nor nor_32 (nor_32_out, not_7_out, nOAM4, not_4_out, not_5_out, not_6_out);
  nor nor_33 (nor_33_out, not_7_out, not_8_out, nOAM5, nOAM6, nOAM7);
  nor nor_34 (nor_34_out, not_7_out, not_8_out, nOAM5, nOAM6, not_6_out);
  nor nor_35 (nor_35_out, not_7_out, not_8_out, nOAM5, not_5_out, nOAM7);
  nor nor_36 (nor_36_out, not_7_out, not_8_out, nOAM5, not_5_out, not_6_out);
  nor nor_37 (nor_37_out, not_7_out, not_8_out, not_4_out, nOAM6, nOAM7);
  nor nor_38 (nor_38_out, not_7_out, not_8_out, not_4_out, nOAM6, not_6_out);
  nor nor_39 (nor_39_out, not_7_out, not_8_out, not_4_out, not_5_out, nOAM7);
  nor nor_40 (nor_40_out, not_7_out, not_8_out, not_4_out, not_5_out, not_6_out);
endmodule

module OAM_CELL (
  input  enable,
  input  in,
  output nout
);

  wire d_ff_1_qn;

  D_Flip_Flop #(.trigger("high")) d_ff_1 (.clk(enable), .D(in), .Qn(d_ff_1_qn));  // open: Q, preset, en, reset
  assign nout = enable ? d_ff_1_qn : 1'bz;  // Controlled_Buffer controlled_buffer_1
endmodule

module OAM_BIG_ROW (
  input  PCLK,
  input  in_2,
  input  in_3,
  input  in_4,
  input  in_5,
  input  in_6,
  input  in_7,
  input  in_8,
  input  in_9,
  input  in_10,
  input  in_11,
  input  in_12,
  input  in_13,
  input  in_14,
  input  in_15,
  input  in_16,
  input  in_17,
  input  in_18,
  input  in_19,
  input  in_20,
  input  in_21,
  input  in_22,
  input  in_23,
  input  in_24,
  input  in_25,
  input  in_26,
  input  in_27,
  input  in_28,
  input  in_29,
  input  in_30,
  input  in_31,
  input  in_32,
  input  in_33,
  input  in_34,
  input  in_35,
  input  in_36,
  input  in_37,
  input  in_38,
  input  in_39,
  input  in_40,
  input  in_41,
  input  in_42,
  input  in_43,
  output out_44
);

  wire controlled_buffer_1_out, controlled_buffer_2_out, controlled_buffer_3_out, controlled_buffer_5_out,
       controlled_buffer_7_out, controlled_buffer_9_out, controlled_buffer_11_out, controlled_buffer_13_out,
       controlled_buffer_15_out, controlled_buffer_17_out, multiplexer_1_out, multiplexer_2_out,
       multiplexer_3_out, multiplexer_4_out, multiplexer_5_out, multiplexer_6_out, multiplexer_7_out,
       multiplexer_8_out, multiplexer_9_out, multiplexer_10_out, oam_cell_1_nout, oam_cell_3_nout,
       oam_cell_5_nout, oam_cell_7_nout, oam_cell_9_nout, oam_cell_11_nout, oam_cell_13_nout,
       oam_cell_15_nout, oam_cell_17_nout;

  Multiplexer multiplexer_1 (.in0(in_2), .in1(1'b0), .out(multiplexer_1_out), .sel(PCLK));  // open: en
  Multiplexer multiplexer_2 (.in0(in_3), .in1(1'b0), .out(multiplexer_2_out), .sel(PCLK));  // open: en
  Multiplexer multiplexer_3 (.in0(in_4), .in1(1'b0), .out(multiplexer_3_out), .sel(PCLK));  // open: en
  Multiplexer multiplexer_4 (.in0(in_5), .in1(1'b0), .out(multiplexer_4_out), .sel(PCLK));  // open: en
  Multiplexer multiplexer_5 (.in0(in_6), .in1(1'b0), .out(multiplexer_5_out), .sel(PCLK));  // open: en
  Multiplexer multiplexer_6 (.in0(in_7), .in1(1'b0), .out(multiplexer_6_out), .sel(PCLK));  // open: en
  Multiplexer multiplexer_7 (.in0(in_8), .in1(1'b0), .out(multiplexer_7_out), .sel(PCLK));  // open: en
  Multiplexer multiplexer_8 (.in0(in_9), .in1(1'b0), .out(multiplexer_8_out), .sel(PCLK));  // open: en
  Multiplexer multiplexer_9 (.in0(in_10), .in1(1'b0), .out(multiplexer_9_out), .sel(PCLK));  // open: en
  Multiplexer multiplexer_10 (.in0(in_43), .in1(1'b1), .out(multiplexer_10_out), .sel(PCLK));  // open: en
  assign controlled_buffer_1_out = multiplexer_1_out ? multiplexer_10_out : 1'bz;  // Controlled_Buffer controlled_buffer_1
  assign controlled_buffer_2_out = multiplexer_1_out ? oam_cell_1_nout : 1'bz;  // Controlled_Buffer controlled_buffer_2
  assign controlled_buffer_3_out = multiplexer_2_out ? multiplexer_10_out : 1'bz;  // Controlled_Buffer controlled_buffer_3
  assign controlled_buffer_2_out = multiplexer_2_out ? oam_cell_3_nout : 1'bz;  // Controlled_Buffer controlled_buffer_4
  assign controlled_buffer_5_out = multiplexer_3_out ? multiplexer_10_out : 1'bz;  // Controlled_Buffer controlled_buffer_5
  assign controlled_buffer_2_out = multiplexer_3_out ? oam_cell_5_nout : 1'bz;  // Controlled_Buffer controlled_buffer_6
  assign controlled_buffer_7_out = multiplexer_4_out ? multiplexer_10_out : 1'bz;  // Controlled_Buffer controlled_buffer_7
  assign controlled_buffer_2_out = multiplexer_4_out ? oam_cell_7_nout : 1'bz;  // Controlled_Buffer controlled_buffer_8
  assign controlled_buffer_9_out = multiplexer_5_out ? multiplexer_10_out : 1'bz;  // Controlled_Buffer controlled_buffer_9
  assign controlled_buffer_2_out = multiplexer_5_out ? oam_cell_9_nout : 1'bz;  // Controlled_Buffer controlled_buffer_10
  assign controlled_buffer_11_out = multiplexer_6_out ? multiplexer_10_out : 1'bz;  // Controlled_Buffer controlled_buffer_11
  assign controlled_buffer_2_out = multiplexer_6_out ? oam_cell_11_nout : 1'bz;  // Controlled_Buffer controlled_buffer_12
  assign controlled_buffer_13_out = multiplexer_7_out ? multiplexer_10_out : 1'bz;  // Controlled_Buffer controlled_buffer_13
  assign controlled_buffer_2_out = multiplexer_7_out ? oam_cell_13_nout : 1'bz;  // Controlled_Buffer controlled_buffer_14
  assign controlled_buffer_15_out = multiplexer_8_out ? multiplexer_10_out : 1'bz;  // Controlled_Buffer controlled_buffer_15
  assign controlled_buffer_2_out = multiplexer_8_out ? oam_cell_15_nout : 1'bz;  // Controlled_Buffer controlled_buffer_16
  assign controlled_buffer_17_out = multiplexer_9_out ? multiplexer_10_out : 1'bz;  // Controlled_Buffer controlled_buffer_17
  assign controlled_buffer_2_out = multiplexer_9_out ? oam_cell_17_nout : 1'bz;  // Controlled_Buffer controlled_buffer_18
  Multiplexer multiplexer_11 (.in0(controlled_buffer_2_out), .in1(1'b1), .out(out_44), .sel(PCLK));  // open: en
  OAM_CELL oam_cell_1 (.enable(in_11), .in(controlled_buffer_1_out), .nout(oam_cell_1_nout));
  OAM_CELL oam_cell_2 (.enable(in_12), .in(controlled_buffer_1_out), .nout(oam_cell_1_nout));
  OAM_CELL oam_cell_3 (.enable(in_11), .in(controlled_buffer_3_out), .nout(oam_cell_3_nout));
  OAM_CELL oam_cell_4 (.enable(in_12), .in(controlled_buffer_3_out), .nout(oam_cell_3_nout));
  OAM_CELL oam_cell_5 (.enable(in_11), .in(controlled_buffer_5_out), .nout(oam_cell_5_nout));
  OAM_CELL oam_cell_6 (.enable(in_12), .in(controlled_buffer_5_out), .nout(oam_cell_5_nout));
  OAM_CELL oam_cell_7 (.enable(in_11), .in(controlled_buffer_7_out), .nout(oam_cell_7_nout));
  OAM_CELL oam_cell_8 (.enable(in_12), .in(controlled_buffer_7_out), .nout(oam_cell_7_nout));
  OAM_CELL oam_cell_9 (.enable(in_11), .in(controlled_buffer_9_out), .nout(oam_cell_9_nout));
  OAM_CELL oam_cell_10 (.enable(in_12), .in(controlled_buffer_9_out), .nout(oam_cell_9_nout));
  OAM_CELL oam_cell_11 (.enable(in_12), .in(controlled_buffer_11_out), .nout(oam_cell_11_nout));
  OAM_CELL oam_cell_12 (.enable(in_11), .in(controlled_buffer_11_out), .nout(oam_cell_11_nout));
  OAM_CELL oam_cell_13 (.enable(in_11), .in(controlled_buffer_13_out), .nout(oam_cell_13_nout));
  OAM_CELL oam_cell_14 (.enable(in_12), .in(controlled_buffer_13_out), .nout(oam_cell_13_nout));
  OAM_CELL oam_cell_15 (.enable(in_11), .in(controlled_buffer_15_out), .nout(oam_cell_15_nout));
  OAM_CELL oam_cell_16 (.enable(in_12), .in(controlled_buffer_15_out), .nout(oam_cell_15_nout));
  OAM_CELL oam_cell_17 (.enable(in_12), .in(controlled_buffer_17_out), .nout(oam_cell_17_nout));
  OAM_CELL oam_cell_18 (.enable(in_11), .in(controlled_buffer_17_out), .nout(oam_cell_17_nout));
  OAM_CELL oam_cell_19 (.enable(in_13), .in(controlled_buffer_1_out), .nout(oam_cell_1_nout));
  OAM_CELL oam_cell_20 (.enable(in_13), .in(controlled_buffer_3_out), .nout(oam_cell_3_nout));
  OAM_CELL oam_cell_21 (.enable(in_13), .in(controlled_buffer_5_out), .nout(oam_cell_5_nout));
  OAM_CELL oam_cell_22 (.enable(in_13), .in(controlled_buffer_7_out), .nout(oam_cell_7_nout));
  OAM_CELL oam_cell_23 (.enable(in_13), .in(controlled_buffer_9_out), .nout(oam_cell_9_nout));
  OAM_CELL oam_cell_24 (.enable(in_13), .in(controlled_buffer_11_out), .nout(oam_cell_11_nout));
  OAM_CELL oam_cell_25 (.enable(in_13), .in(controlled_buffer_13_out), .nout(oam_cell_13_nout));
  OAM_CELL oam_cell_26 (.enable(in_13), .in(controlled_buffer_15_out), .nout(oam_cell_15_nout));
  OAM_CELL oam_cell_27 (.enable(in_13), .in(controlled_buffer_17_out), .nout(oam_cell_17_nout));
  OAM_CELL oam_cell_28 (.enable(in_14), .in(controlled_buffer_1_out), .nout(oam_cell_1_nout));
  OAM_CELL oam_cell_29 (.enable(in_14), .in(controlled_buffer_3_out), .nout(oam_cell_3_nout));
  OAM_CELL oam_cell_30 (.enable(in_14), .in(controlled_buffer_5_out), .nout(oam_cell_5_nout));
  OAM_CELL oam_cell_31 (.enable(in_14), .in(controlled_buffer_7_out), .nout(oam_cell_7_nout));
  OAM_CELL oam_cell_32 (.enable(in_14), .in(controlled_buffer_9_out), .nout(oam_cell_9_nout));
  OAM_CELL oam_cell_33 (.enable(in_14), .in(controlled_buffer_11_out), .nout(oam_cell_11_nout));
  OAM_CELL oam_cell_34 (.enable(in_14), .in(controlled_buffer_13_out), .nout(oam_cell_13_nout));
  OAM_CELL oam_cell_35 (.enable(in_14), .in(controlled_buffer_15_out), .nout(oam_cell_15_nout));
  OAM_CELL oam_cell_36 (.enable(in_14), .in(controlled_buffer_17_out), .nout(oam_cell_17_nout));
  OAM_CELL oam_cell_37 (.enable(in_15), .in(controlled_buffer_1_out), .nout(oam_cell_1_nout));
  OAM_CELL oam_cell_38 (.enable(in_15), .in(controlled_buffer_3_out), .nout(oam_cell_3_nout));
  OAM_CELL oam_cell_39 (.enable(in_15), .in(controlled_buffer_5_out), .nout(oam_cell_5_nout));
  OAM_CELL oam_cell_40 (.enable(in_15), .in(controlled_buffer_7_out), .nout(oam_cell_7_nout));
  OAM_CELL oam_cell_41 (.enable(in_15), .in(controlled_buffer_9_out), .nout(oam_cell_9_nout));
  OAM_CELL oam_cell_42 (.enable(in_15), .in(controlled_buffer_11_out), .nout(oam_cell_11_nout));
  OAM_CELL oam_cell_43 (.enable(in_15), .in(controlled_buffer_13_out), .nout(oam_cell_13_nout));
  OAM_CELL oam_cell_44 (.enable(in_15), .in(controlled_buffer_15_out), .nout(oam_cell_15_nout));
  OAM_CELL oam_cell_45 (.enable(in_15), .in(controlled_buffer_17_out), .nout(oam_cell_17_nout));
  OAM_CELL oam_cell_46 (.enable(in_16), .in(controlled_buffer_1_out), .nout(oam_cell_1_nout));
  OAM_CELL oam_cell_47 (.enable(in_16), .in(controlled_buffer_3_out), .nout(oam_cell_3_nout));
  OAM_CELL oam_cell_48 (.enable(in_16), .in(controlled_buffer_5_out), .nout(oam_cell_5_nout));
  OAM_CELL oam_cell_49 (.enable(in_16), .in(controlled_buffer_7_out), .nout(oam_cell_7_nout));
  OAM_CELL oam_cell_50 (.enable(in_16), .in(controlled_buffer_9_out), .nout(oam_cell_9_nout));
  OAM_CELL oam_cell_51 (.enable(in_16), .in(controlled_buffer_11_out), .nout(oam_cell_11_nout));
  OAM_CELL oam_cell_52 (.enable(in_16), .in(controlled_buffer_13_out), .nout(oam_cell_13_nout));
  OAM_CELL oam_cell_53 (.enable(in_16), .in(controlled_buffer_15_out), .nout(oam_cell_15_nout));
  OAM_CELL oam_cell_54 (.enable(in_16), .in(controlled_buffer_17_out), .nout(oam_cell_17_nout));
  OAM_CELL oam_cell_55 (.enable(in_17), .in(controlled_buffer_1_out), .nout(oam_cell_1_nout));
  OAM_CELL oam_cell_56 (.enable(in_17), .in(controlled_buffer_3_out), .nout(oam_cell_3_nout));
  OAM_CELL oam_cell_57 (.enable(in_17), .in(controlled_buffer_5_out), .nout(oam_cell_5_nout));
  OAM_CELL oam_cell_58 (.enable(in_17), .in(controlled_buffer_7_out), .nout(oam_cell_7_nout));
  OAM_CELL oam_cell_59 (.enable(in_17), .in(controlled_buffer_9_out), .nout(oam_cell_9_nout));
  OAM_CELL oam_cell_60 (.enable(in_17), .in(controlled_buffer_11_out), .nout(oam_cell_11_nout));
  OAM_CELL oam_cell_61 (.enable(in_17), .in(controlled_buffer_13_out), .nout(oam_cell_13_nout));
  OAM_CELL oam_cell_62 (.enable(in_17), .in(controlled_buffer_15_out), .nout(oam_cell_15_nout));
  OAM_CELL oam_cell_63 (.enable(in_17), .in(controlled_buffer_17_out), .nout(oam_cell_17_nout));
  OAM_CELL oam_cell_64 (.enable(in_18), .in(controlled_buffer_1_out), .nout(oam_cell_1_nout));
  OAM_CELL oam_cell_65 (.enable(in_18), .in(controlled_buffer_3_out), .nout(oam_cell_3_nout));
  OAM_CELL oam_cell_66 (.enable(in_18), .in(controlled_buffer_5_out), .nout(oam_cell_5_nout));
  OAM_CELL oam_cell_67 (.enable(in_18), .in(controlled_buffer_7_out), .nout(oam_cell_7_nout));
  OAM_CELL oam_cell_68 (.enable(in_18), .in(controlled_buffer_9_out), .nout(oam_cell_9_nout));
  OAM_CELL oam_cell_69 (.enable(in_18), .in(controlled_buffer_11_out), .nout(oam_cell_11_nout));
  OAM_CELL oam_cell_70 (.enable(in_18), .in(controlled_buffer_13_out), .nout(oam_cell_13_nout));
  OAM_CELL oam_cell_71 (.enable(in_18), .in(controlled_buffer_15_out), .nout(oam_cell_15_nout));
  OAM_CELL oam_cell_72 (.enable(in_18), .in(controlled_buffer_17_out), .nout(oam_cell_17_nout));
  OAM_CELL oam_cell_73 (.enable(in_19), .in(controlled_buffer_1_out), .nout(oam_cell_1_nout));
  OAM_CELL oam_cell_74 (.enable(in_20), .in(controlled_buffer_1_out), .nout(oam_cell_1_nout));
  OAM_CELL oam_cell_75 (.enable(in_19), .in(controlled_buffer_3_out), .nout(oam_cell_3_nout));
  OAM_CELL oam_cell_76 (.enable(in_20), .in(controlled_buffer_3_out), .nout(oam_cell_3_nout));
  OAM_CELL oam_cell_77 (.enable(in_19), .in(controlled_buffer_5_out), .nout(oam_cell_5_nout));
  OAM_CELL oam_cell_78 (.enable(in_20), .in(controlled_buffer_5_out), .nout(oam_cell_5_nout));
  OAM_CELL oam_cell_79 (.enable(in_20), .in(controlled_buffer_7_out), .nout(oam_cell_7_nout));
  OAM_CELL oam_cell_80 (.enable(in_19), .in(controlled_buffer_7_out), .nout(oam_cell_7_nout));
  OAM_CELL oam_cell_81 (.enable(in_20), .in(controlled_buffer_9_out), .nout(oam_cell_9_nout));
  OAM_CELL oam_cell_82 (.enable(in_19), .in(controlled_buffer_9_out), .nout(oam_cell_9_nout));
  OAM_CELL oam_cell_83 (.enable(in_20), .in(controlled_buffer_11_out), .nout(oam_cell_11_nout));
  OAM_CELL oam_cell_84 (.enable(in_19), .in(controlled_buffer_11_out), .nout(oam_cell_11_nout));
  OAM_CELL oam_cell_85 (.enable(in_20), .in(controlled_buffer_13_out), .nout(oam_cell_13_nout));
  OAM_CELL oam_cell_86 (.enable(in_19), .in(controlled_buffer_13_out), .nout(oam_cell_13_nout));
  OAM_CELL oam_cell_87 (.enable(in_19), .in(controlled_buffer_15_out), .nout(oam_cell_15_nout));
  OAM_CELL oam_cell_88 (.enable(in_20), .in(controlled_buffer_15_out), .nout(oam_cell_15_nout));
  OAM_CELL oam_cell_89 (.enable(in_19), .in(controlled_buffer_17_out), .nout(oam_cell_17_nout));
  OAM_CELL oam_cell_90 (.enable(in_20), .in(controlled_buffer_17_out), .nout(oam_cell_17_nout));
  OAM_CELL oam_cell_91 (.enable(in_21), .in(controlled_buffer_1_out), .nout(oam_cell_1_nout));
  OAM_CELL oam_cell_92 (.enable(in_21), .in(controlled_buffer_3_out), .nout(oam_cell_3_nout));
  OAM_CELL oam_cell_93 (.enable(in_21), .in(controlled_buffer_5_out), .nout(oam_cell_5_nout));
  OAM_CELL oam_cell_94 (.enable(in_21), .in(controlled_buffer_7_out), .nout(oam_cell_7_nout));
  OAM_CELL oam_cell_95 (.enable(in_21), .in(controlled_buffer_9_out), .nout(oam_cell_9_nout));
  OAM_CELL oam_cell_96 (.enable(in_21), .in(controlled_buffer_11_out), .nout(oam_cell_11_nout));
  OAM_CELL oam_cell_97 (.enable(in_21), .in(controlled_buffer_13_out), .nout(oam_cell_13_nout));
  OAM_CELL oam_cell_98 (.enable(in_21), .in(controlled_buffer_15_out), .nout(oam_cell_15_nout));
  OAM_CELL oam_cell_99 (.enable(in_21), .in(controlled_buffer_17_out), .nout(oam_cell_17_nout));
  OAM_CELL oam_cell_100 (.enable(in_22), .in(controlled_buffer_1_out), .nout(oam_cell_1_nout));
  OAM_CELL oam_cell_101 (.enable(in_22), .in(controlled_buffer_3_out), .nout(oam_cell_3_nout));
  OAM_CELL oam_cell_102 (.enable(in_22), .in(controlled_buffer_5_out), .nout(oam_cell_5_nout));
  OAM_CELL oam_cell_103 (.enable(in_22), .in(controlled_buffer_7_out), .nout(oam_cell_7_nout));
  OAM_CELL oam_cell_104 (.enable(in_22), .in(controlled_buffer_9_out), .nout(oam_cell_9_nout));
  OAM_CELL oam_cell_105 (.enable(in_22), .in(controlled_buffer_11_out), .nout(oam_cell_11_nout));
  OAM_CELL oam_cell_106 (.enable(in_22), .in(controlled_buffer_13_out), .nout(oam_cell_13_nout));
  OAM_CELL oam_cell_107 (.enable(in_22), .in(controlled_buffer_15_out), .nout(oam_cell_15_nout));
  OAM_CELL oam_cell_108 (.enable(in_22), .in(controlled_buffer_17_out), .nout(oam_cell_17_nout));
  OAM_CELL oam_cell_109 (.enable(in_23), .in(controlled_buffer_1_out), .nout(oam_cell_1_nout));
  OAM_CELL oam_cell_110 (.enable(in_23), .in(controlled_buffer_3_out), .nout(oam_cell_3_nout));
  OAM_CELL oam_cell_111 (.enable(in_23), .in(controlled_buffer_5_out), .nout(oam_cell_5_nout));
  OAM_CELL oam_cell_112 (.enable(in_23), .in(controlled_buffer_7_out), .nout(oam_cell_7_nout));
  OAM_CELL oam_cell_113 (.enable(in_23), .in(controlled_buffer_9_out), .nout(oam_cell_9_nout));
  OAM_CELL oam_cell_114 (.enable(in_23), .in(controlled_buffer_11_out), .nout(oam_cell_11_nout));
  OAM_CELL oam_cell_115 (.enable(in_23), .in(controlled_buffer_13_out), .nout(oam_cell_13_nout));
  OAM_CELL oam_cell_116 (.enable(in_23), .in(controlled_buffer_15_out), .nout(oam_cell_15_nout));
  OAM_CELL oam_cell_117 (.enable(in_23), .in(controlled_buffer_17_out), .nout(oam_cell_17_nout));
  OAM_CELL oam_cell_118 (.enable(in_24), .in(controlled_buffer_1_out), .nout(oam_cell_1_nout));
  OAM_CELL oam_cell_119 (.enable(in_24), .in(controlled_buffer_3_out), .nout(oam_cell_3_nout));
  OAM_CELL oam_cell_120 (.enable(in_24), .in(controlled_buffer_5_out), .nout(oam_cell_5_nout));
  OAM_CELL oam_cell_121 (.enable(in_24), .in(controlled_buffer_7_out), .nout(oam_cell_7_nout));
  OAM_CELL oam_cell_122 (.enable(in_24), .in(controlled_buffer_9_out), .nout(oam_cell_9_nout));
  OAM_CELL oam_cell_123 (.enable(in_24), .in(controlled_buffer_11_out), .nout(oam_cell_11_nout));
  OAM_CELL oam_cell_124 (.enable(in_24), .in(controlled_buffer_13_out), .nout(oam_cell_13_nout));
  OAM_CELL oam_cell_125 (.enable(in_24), .in(controlled_buffer_15_out), .nout(oam_cell_15_nout));
  OAM_CELL oam_cell_126 (.enable(in_24), .in(controlled_buffer_17_out), .nout(oam_cell_17_nout));
  OAM_CELL oam_cell_127 (.enable(in_25), .in(controlled_buffer_1_out), .nout(oam_cell_1_nout));
  OAM_CELL oam_cell_128 (.enable(in_25), .in(controlled_buffer_3_out), .nout(oam_cell_3_nout));
  OAM_CELL oam_cell_129 (.enable(in_25), .in(controlled_buffer_5_out), .nout(oam_cell_5_nout));
  OAM_CELL oam_cell_130 (.enable(in_25), .in(controlled_buffer_7_out), .nout(oam_cell_7_nout));
  OAM_CELL oam_cell_131 (.enable(in_25), .in(controlled_buffer_9_out), .nout(oam_cell_9_nout));
  OAM_CELL oam_cell_132 (.enable(in_25), .in(controlled_buffer_11_out), .nout(oam_cell_11_nout));
  OAM_CELL oam_cell_133 (.enable(in_25), .in(controlled_buffer_13_out), .nout(oam_cell_13_nout));
  OAM_CELL oam_cell_134 (.enable(in_25), .in(controlled_buffer_15_out), .nout(oam_cell_15_nout));
  OAM_CELL oam_cell_135 (.enable(in_25), .in(controlled_buffer_17_out), .nout(oam_cell_17_nout));
  OAM_CELL oam_cell_136 (.enable(in_26), .in(controlled_buffer_1_out), .nout(oam_cell_1_nout));
  OAM_CELL oam_cell_137 (.enable(in_26), .in(controlled_buffer_3_out), .nout(oam_cell_3_nout));
  OAM_CELL oam_cell_138 (.enable(in_26), .in(controlled_buffer_5_out), .nout(oam_cell_5_nout));
  OAM_CELL oam_cell_139 (.enable(in_26), .in(controlled_buffer_7_out), .nout(oam_cell_7_nout));
  OAM_CELL oam_cell_140 (.enable(in_26), .in(controlled_buffer_9_out), .nout(oam_cell_9_nout));
  OAM_CELL oam_cell_141 (.enable(in_26), .in(controlled_buffer_11_out), .nout(oam_cell_11_nout));
  OAM_CELL oam_cell_142 (.enable(in_26), .in(controlled_buffer_13_out), .nout(oam_cell_13_nout));
  OAM_CELL oam_cell_143 (.enable(in_26), .in(controlled_buffer_15_out), .nout(oam_cell_15_nout));
  OAM_CELL oam_cell_144 (.enable(in_26), .in(controlled_buffer_17_out), .nout(oam_cell_17_nout));
  OAM_CELL oam_cell_145 (.enable(in_28), .in(controlled_buffer_1_out), .nout(oam_cell_1_nout));
  OAM_CELL oam_cell_146 (.enable(in_27), .in(controlled_buffer_1_out), .nout(oam_cell_1_nout));
  OAM_CELL oam_cell_147 (.enable(in_27), .in(controlled_buffer_3_out), .nout(oam_cell_3_nout));
  OAM_CELL oam_cell_148 (.enable(in_28), .in(controlled_buffer_3_out), .nout(oam_cell_3_nout));
  OAM_CELL oam_cell_149 (.enable(in_28), .in(controlled_buffer_5_out), .nout(oam_cell_5_nout));
  OAM_CELL oam_cell_150 (.enable(in_27), .in(controlled_buffer_5_out), .nout(oam_cell_5_nout));
  OAM_CELL oam_cell_151 (.enable(in_28), .in(controlled_buffer_7_out), .nout(oam_cell_7_nout));
  OAM_CELL oam_cell_152 (.enable(in_27), .in(controlled_buffer_7_out), .nout(oam_cell_7_nout));
  OAM_CELL oam_cell_153 (.enable(in_28), .in(controlled_buffer_9_out), .nout(oam_cell_9_nout));
  OAM_CELL oam_cell_154 (.enable(in_27), .in(controlled_buffer_9_out), .nout(oam_cell_9_nout));
  OAM_CELL oam_cell_155 (.enable(in_27), .in(controlled_buffer_11_out), .nout(oam_cell_11_nout));
  OAM_CELL oam_cell_156 (.enable(in_28), .in(controlled_buffer_11_out), .nout(oam_cell_11_nout));
  OAM_CELL oam_cell_157 (.enable(in_27), .in(controlled_buffer_13_out), .nout(oam_cell_13_nout));
  OAM_CELL oam_cell_158 (.enable(in_28), .in(controlled_buffer_13_out), .nout(oam_cell_13_nout));
  OAM_CELL oam_cell_159 (.enable(in_27), .in(controlled_buffer_15_out), .nout(oam_cell_15_nout));
  OAM_CELL oam_cell_160 (.enable(in_28), .in(controlled_buffer_15_out), .nout(oam_cell_15_nout));
  OAM_CELL oam_cell_161 (.enable(in_28), .in(controlled_buffer_17_out), .nout(oam_cell_17_nout));
  OAM_CELL oam_cell_162 (.enable(in_27), .in(controlled_buffer_17_out), .nout(oam_cell_17_nout));
  OAM_CELL oam_cell_163 (.enable(in_29), .in(controlled_buffer_1_out), .nout(oam_cell_1_nout));
  OAM_CELL oam_cell_164 (.enable(in_29), .in(controlled_buffer_3_out), .nout(oam_cell_3_nout));
  OAM_CELL oam_cell_165 (.enable(in_29), .in(controlled_buffer_5_out), .nout(oam_cell_5_nout));
  OAM_CELL oam_cell_166 (.enable(in_29), .in(controlled_buffer_7_out), .nout(oam_cell_7_nout));
  OAM_CELL oam_cell_167 (.enable(in_29), .in(controlled_buffer_9_out), .nout(oam_cell_9_nout));
  OAM_CELL oam_cell_168 (.enable(in_29), .in(controlled_buffer_11_out), .nout(oam_cell_11_nout));
  OAM_CELL oam_cell_169 (.enable(in_29), .in(controlled_buffer_13_out), .nout(oam_cell_13_nout));
  OAM_CELL oam_cell_170 (.enable(in_29), .in(controlled_buffer_15_out), .nout(oam_cell_15_nout));
  OAM_CELL oam_cell_171 (.enable(in_29), .in(controlled_buffer_17_out), .nout(oam_cell_17_nout));
  OAM_CELL oam_cell_172 (.enable(in_30), .in(controlled_buffer_1_out), .nout(oam_cell_1_nout));
  OAM_CELL oam_cell_173 (.enable(in_30), .in(controlled_buffer_3_out), .nout(oam_cell_3_nout));
  OAM_CELL oam_cell_174 (.enable(in_30), .in(controlled_buffer_5_out), .nout(oam_cell_5_nout));
  OAM_CELL oam_cell_175 (.enable(in_30), .in(controlled_buffer_7_out), .nout(oam_cell_7_nout));
  OAM_CELL oam_cell_176 (.enable(in_30), .in(controlled_buffer_9_out), .nout(oam_cell_9_nout));
  OAM_CELL oam_cell_177 (.enable(in_30), .in(controlled_buffer_11_out), .nout(oam_cell_11_nout));
  OAM_CELL oam_cell_178 (.enable(in_30), .in(controlled_buffer_13_out), .nout(oam_cell_13_nout));
  OAM_CELL oam_cell_179 (.enable(in_30), .in(controlled_buffer_15_out), .nout(oam_cell_15_nout));
  OAM_CELL oam_cell_180 (.enable(in_30), .in(controlled_buffer_17_out), .nout(oam_cell_17_nout));
  OAM_CELL oam_cell_181 (.enable(in_31), .in(controlled_buffer_1_out), .nout(oam_cell_1_nout));
  OAM_CELL oam_cell_182 (.enable(in_31), .in(controlled_buffer_3_out), .nout(oam_cell_3_nout));
  OAM_CELL oam_cell_183 (.enable(in_31), .in(controlled_buffer_5_out), .nout(oam_cell_5_nout));
  OAM_CELL oam_cell_184 (.enable(in_31), .in(controlled_buffer_7_out), .nout(oam_cell_7_nout));
  OAM_CELL oam_cell_185 (.enable(in_31), .in(controlled_buffer_9_out), .nout(oam_cell_9_nout));
  OAM_CELL oam_cell_186 (.enable(in_31), .in(controlled_buffer_11_out), .nout(oam_cell_11_nout));
  OAM_CELL oam_cell_187 (.enable(in_31), .in(controlled_buffer_13_out), .nout(oam_cell_13_nout));
  OAM_CELL oam_cell_188 (.enable(in_31), .in(controlled_buffer_15_out), .nout(oam_cell_15_nout));
  OAM_CELL oam_cell_189 (.enable(in_31), .in(controlled_buffer_17_out), .nout(oam_cell_17_nout));
  OAM_CELL oam_cell_190 (.enable(in_32), .in(controlled_buffer_1_out), .nout(oam_cell_1_nout));
  OAM_CELL oam_cell_191 (.enable(in_32), .in(controlled_buffer_3_out), .nout(oam_cell_3_nout));
  OAM_CELL oam_cell_192 (.enable(in_32), .in(controlled_buffer_5_out), .nout(oam_cell_5_nout));
  OAM_CELL oam_cell_193 (.enable(in_32), .in(controlled_buffer_7_out), .nout(oam_cell_7_nout));
  OAM_CELL oam_cell_194 (.enable(in_32), .in(controlled_buffer_9_out), .nout(oam_cell_9_nout));
  OAM_CELL oam_cell_195 (.enable(in_32), .in(controlled_buffer_11_out), .nout(oam_cell_11_nout));
  OAM_CELL oam_cell_196 (.enable(in_32), .in(controlled_buffer_13_out), .nout(oam_cell_13_nout));
  OAM_CELL oam_cell_197 (.enable(in_32), .in(controlled_buffer_15_out), .nout(oam_cell_15_nout));
  OAM_CELL oam_cell_198 (.enable(in_32), .in(controlled_buffer_17_out), .nout(oam_cell_17_nout));
  OAM_CELL oam_cell_199 (.enable(in_33), .in(controlled_buffer_1_out), .nout(oam_cell_1_nout));
  OAM_CELL oam_cell_200 (.enable(in_33), .in(controlled_buffer_3_out), .nout(oam_cell_3_nout));
  OAM_CELL oam_cell_201 (.enable(in_33), .in(controlled_buffer_5_out), .nout(oam_cell_5_nout));
  OAM_CELL oam_cell_202 (.enable(in_33), .in(controlled_buffer_7_out), .nout(oam_cell_7_nout));
  OAM_CELL oam_cell_203 (.enable(in_33), .in(controlled_buffer_9_out), .nout(oam_cell_9_nout));
  OAM_CELL oam_cell_204 (.enable(in_33), .in(controlled_buffer_11_out), .nout(oam_cell_11_nout));
  OAM_CELL oam_cell_205 (.enable(in_33), .in(controlled_buffer_13_out), .nout(oam_cell_13_nout));
  OAM_CELL oam_cell_206 (.enable(in_33), .in(controlled_buffer_15_out), .nout(oam_cell_15_nout));
  OAM_CELL oam_cell_207 (.enable(in_33), .in(controlled_buffer_17_out), .nout(oam_cell_17_nout));
  OAM_CELL oam_cell_208 (.enable(in_34), .in(controlled_buffer_1_out), .nout(oam_cell_1_nout));
  OAM_CELL oam_cell_209 (.enable(in_34), .in(controlled_buffer_3_out), .nout(oam_cell_3_nout));
  OAM_CELL oam_cell_210 (.enable(in_34), .in(controlled_buffer_5_out), .nout(oam_cell_5_nout));
  OAM_CELL oam_cell_211 (.enable(in_34), .in(controlled_buffer_7_out), .nout(oam_cell_7_nout));
  OAM_CELL oam_cell_212 (.enable(in_34), .in(controlled_buffer_9_out), .nout(oam_cell_9_nout));
  OAM_CELL oam_cell_213 (.enable(in_34), .in(controlled_buffer_11_out), .nout(oam_cell_11_nout));
  OAM_CELL oam_cell_214 (.enable(in_34), .in(controlled_buffer_13_out), .nout(oam_cell_13_nout));
  OAM_CELL oam_cell_215 (.enable(in_34), .in(controlled_buffer_15_out), .nout(oam_cell_15_nout));
  OAM_CELL oam_cell_216 (.enable(in_34), .in(controlled_buffer_17_out), .nout(oam_cell_17_nout));
  OAM_CELL oam_cell_217 (.enable(in_36), .in(controlled_buffer_1_out), .nout(oam_cell_1_nout));
  OAM_CELL oam_cell_218 (.enable(in_35), .in(controlled_buffer_1_out), .nout(oam_cell_1_nout));
  OAM_CELL oam_cell_219 (.enable(in_35), .in(controlled_buffer_3_out), .nout(oam_cell_3_nout));
  OAM_CELL oam_cell_220 (.enable(in_36), .in(controlled_buffer_3_out), .nout(oam_cell_3_nout));
  OAM_CELL oam_cell_221 (.enable(in_35), .in(controlled_buffer_5_out), .nout(oam_cell_5_nout));
  OAM_CELL oam_cell_222 (.enable(in_36), .in(controlled_buffer_5_out), .nout(oam_cell_5_nout));
  OAM_CELL oam_cell_223 (.enable(in_35), .in(controlled_buffer_7_out), .nout(oam_cell_7_nout));
  OAM_CELL oam_cell_224 (.enable(in_36), .in(controlled_buffer_7_out), .nout(oam_cell_7_nout));
  OAM_CELL oam_cell_225 (.enable(in_36), .in(controlled_buffer_9_out), .nout(oam_cell_9_nout));
  OAM_CELL oam_cell_226 (.enable(in_35), .in(controlled_buffer_9_out), .nout(oam_cell_9_nout));
  OAM_CELL oam_cell_227 (.enable(in_35), .in(controlled_buffer_11_out), .nout(oam_cell_11_nout));
  OAM_CELL oam_cell_228 (.enable(in_36), .in(controlled_buffer_11_out), .nout(oam_cell_11_nout));
  OAM_CELL oam_cell_229 (.enable(in_36), .in(controlled_buffer_13_out), .nout(oam_cell_13_nout));
  OAM_CELL oam_cell_230 (.enable(in_35), .in(controlled_buffer_13_out), .nout(oam_cell_13_nout));
  OAM_CELL oam_cell_231 (.enable(in_36), .in(controlled_buffer_15_out), .nout(oam_cell_15_nout));
  OAM_CELL oam_cell_232 (.enable(in_35), .in(controlled_buffer_15_out), .nout(oam_cell_15_nout));
  OAM_CELL oam_cell_233 (.enable(in_36), .in(controlled_buffer_17_out), .nout(oam_cell_17_nout));
  OAM_CELL oam_cell_234 (.enable(in_35), .in(controlled_buffer_17_out), .nout(oam_cell_17_nout));
  OAM_CELL oam_cell_235 (.enable(in_37), .in(controlled_buffer_1_out), .nout(oam_cell_1_nout));
  OAM_CELL oam_cell_236 (.enable(in_37), .in(controlled_buffer_3_out), .nout(oam_cell_3_nout));
  OAM_CELL oam_cell_237 (.enable(in_37), .in(controlled_buffer_5_out), .nout(oam_cell_5_nout));
  OAM_CELL oam_cell_238 (.enable(in_37), .in(controlled_buffer_7_out), .nout(oam_cell_7_nout));
  OAM_CELL oam_cell_239 (.enable(in_37), .in(controlled_buffer_9_out), .nout(oam_cell_9_nout));
  OAM_CELL oam_cell_240 (.enable(in_37), .in(controlled_buffer_11_out), .nout(oam_cell_11_nout));
  OAM_CELL oam_cell_241 (.enable(in_37), .in(controlled_buffer_13_out), .nout(oam_cell_13_nout));
  OAM_CELL oam_cell_242 (.enable(in_37), .in(controlled_buffer_15_out), .nout(oam_cell_15_nout));
  OAM_CELL oam_cell_243 (.enable(in_37), .in(controlled_buffer_17_out), .nout(oam_cell_17_nout));
  OAM_CELL oam_cell_244 (.enable(in_38), .in(controlled_buffer_1_out), .nout(oam_cell_1_nout));
  OAM_CELL oam_cell_245 (.enable(in_38), .in(controlled_buffer_3_out), .nout(oam_cell_3_nout));
  OAM_CELL oam_cell_246 (.enable(in_38), .in(controlled_buffer_5_out), .nout(oam_cell_5_nout));
  OAM_CELL oam_cell_247 (.enable(in_38), .in(controlled_buffer_7_out), .nout(oam_cell_7_nout));
  OAM_CELL oam_cell_248 (.enable(in_38), .in(controlled_buffer_9_out), .nout(oam_cell_9_nout));
  OAM_CELL oam_cell_249 (.enable(in_38), .in(controlled_buffer_11_out), .nout(oam_cell_11_nout));
  OAM_CELL oam_cell_250 (.enable(in_38), .in(controlled_buffer_13_out), .nout(oam_cell_13_nout));
  OAM_CELL oam_cell_251 (.enable(in_38), .in(controlled_buffer_15_out), .nout(oam_cell_15_nout));
  OAM_CELL oam_cell_252 (.enable(in_38), .in(controlled_buffer_17_out), .nout(oam_cell_17_nout));
  OAM_CELL oam_cell_253 (.enable(in_39), .in(controlled_buffer_1_out), .nout(oam_cell_1_nout));
  OAM_CELL oam_cell_254 (.enable(in_39), .in(controlled_buffer_3_out), .nout(oam_cell_3_nout));
  OAM_CELL oam_cell_255 (.enable(in_39), .in(controlled_buffer_5_out), .nout(oam_cell_5_nout));
  OAM_CELL oam_cell_256 (.enable(in_39), .in(controlled_buffer_7_out), .nout(oam_cell_7_nout));
  OAM_CELL oam_cell_257 (.enable(in_39), .in(controlled_buffer_9_out), .nout(oam_cell_9_nout));
  OAM_CELL oam_cell_258 (.enable(in_39), .in(controlled_buffer_11_out), .nout(oam_cell_11_nout));
  OAM_CELL oam_cell_259 (.enable(in_39), .in(controlled_buffer_13_out), .nout(oam_cell_13_nout));
  OAM_CELL oam_cell_260 (.enable(in_39), .in(controlled_buffer_15_out), .nout(oam_cell_15_nout));
  OAM_CELL oam_cell_261 (.enable(in_39), .in(controlled_buffer_17_out), .nout(oam_cell_17_nout));
  OAM_CELL oam_cell_262 (.enable(in_40), .in(controlled_buffer_1_out), .nout(oam_cell_1_nout));
  OAM_CELL oam_cell_263 (.enable(in_40), .in(controlled_buffer_3_out), .nout(oam_cell_3_nout));
  OAM_CELL oam_cell_264 (.enable(in_40), .in(controlled_buffer_5_out), .nout(oam_cell_5_nout));
  OAM_CELL oam_cell_265 (.enable(in_40), .in(controlled_buffer_7_out), .nout(oam_cell_7_nout));
  OAM_CELL oam_cell_266 (.enable(in_40), .in(controlled_buffer_9_out), .nout(oam_cell_9_nout));
  OAM_CELL oam_cell_267 (.enable(in_40), .in(controlled_buffer_11_out), .nout(oam_cell_11_nout));
  OAM_CELL oam_cell_268 (.enable(in_40), .in(controlled_buffer_13_out), .nout(oam_cell_13_nout));
  OAM_CELL oam_cell_269 (.enable(in_40), .in(controlled_buffer_15_out), .nout(oam_cell_15_nout));
  OAM_CELL oam_cell_270 (.enable(in_40), .in(controlled_buffer_17_out), .nout(oam_cell_17_nout));
  OAM_CELL oam_cell_271 (.enable(in_41), .in(controlled_buffer_1_out), .nout(oam_cell_1_nout));
  OAM_CELL oam_cell_272 (.enable(in_41), .in(controlled_buffer_3_out), .nout(oam_cell_3_nout));
  OAM_CELL oam_cell_273 (.enable(in_41), .in(controlled_buffer_5_out), .nout(oam_cell_5_nout));
  OAM_CELL oam_cell_274 (.enable(in_41), .in(controlled_buffer_7_out), .nout(oam_cell_7_nout));
  OAM_CELL oam_cell_275 (.enable(in_41), .in(controlled_buffer_9_out), .nout(oam_cell_9_nout));
  OAM_CELL oam_cell_276 (.enable(in_41), .in(controlled_buffer_11_out), .nout(oam_cell_11_nout));
  OAM_CELL oam_cell_277 (.enable(in_41), .in(controlled_buffer_13_out), .nout(oam_cell_13_nout));
  OAM_CELL oam_cell_278 (.enable(in_41), .in(controlled_buffer_15_out), .nout(oam_cell_15_nout));
  OAM_CELL oam_cell_279 (.enable(in_41), .in(controlled_buffer_17_out), .nout(oam_cell_17_nout));
  OAM_CELL oam_cell_280 (.enable(in_42), .in(controlled_buffer_1_out), .nout(oam_cell_1_nout));
  OAM_CELL oam_cell_281 (.enable(in_42), .in(controlled_buffer_3_out), .nout(oam_cell_3_nout));
  OAM_CELL oam_cell_282 (.enable(in_42), .in(controlled_buffer_5_out), .nout(oam_cell_5_nout));
  OAM_CELL oam_cell_283 (.enable(in_42), .in(controlled_buffer_7_out), .nout(oam_cell_7_nout));
  OAM_CELL oam_cell_284 (.enable(in_42), .in(controlled_buffer_9_out), .nout(oam_cell_9_nout));
  OAM_CELL oam_cell_285 (.enable(in_42), .in(controlled_buffer_11_out), .nout(oam_cell_11_nout));
  OAM_CELL oam_cell_286 (.enable(in_42), .in(controlled_buffer_13_out), .nout(oam_cell_13_nout));
  OAM_CELL oam_cell_287 (.enable(in_42), .in(controlled_buffer_15_out), .nout(oam_cell_15_nout));
  OAM_CELL oam_cell_288 (.enable(in_42), .in(controlled_buffer_17_out), .nout(oam_cell_17_nout));
endmodule

module OAM_SMALL_ROW (
  input  PCLK,
  input  in_2,
  input  in_3,
  input  in_4,
  input  in_5,
  input  in_6,
  input  in_7,
  input  in_8,
  input  in_9,
  input  in_10,
  input  in_11,
  input  in_12,
  input  in_13,
  input  in_14,
  input  in_15,
  input  in_16,
  input  in_17,
  input  in_18,
  input  in_19,
  input  in_20,
  input  in_21,
  input  in_22,
  input  in_23,
  input  in_24,
  input  in_25,
  input  in_26,
  input  in_27,
  input  in_28,
  input  in_29,
  input  in_30,
  input  in_31,
  input  in_32,
  input  in_33,
  input  in_34,
  input  in_35,
  input  in_36,
  input  in_37,
  input  in_38,
  input  in_39,
  input  in_40,
  input  in_41,
  output out_42
);

  wire controlled_buffer_1_out, controlled_buffer_2_out, controlled_buffer_3_out, controlled_buffer_5_out,
       controlled_buffer_7_out, controlled_buffer_9_out, controlled_buffer_11_out, controlled_buffer_13_out,
       multiplexer_1_out, multiplexer_2_out, multiplexer_3_out, multiplexer_4_out, multiplexer_5_out,
       multiplexer_6_out, multiplexer_7_out, multiplexer_8_out, oam_cell_1_nout, oam_cell_3_nout,
       oam_cell_5_nout, oam_cell_7_nout, oam_cell_9_nout, oam_cell_11_nout, oam_cell_13_nout;

  Multiplexer multiplexer_1 (.in0(in_2), .in1(1'b0), .out(multiplexer_1_out), .sel(PCLK));  // open: en
  Multiplexer multiplexer_2 (.in0(in_3), .in1(1'b0), .out(multiplexer_2_out), .sel(PCLK));  // open: en
  Multiplexer multiplexer_3 (.in0(in_4), .in1(1'b0), .out(multiplexer_3_out), .sel(PCLK));  // open: en
  Multiplexer multiplexer_4 (.in0(in_5), .in1(1'b0), .out(multiplexer_4_out), .sel(PCLK));  // open: en
  Multiplexer multiplexer_5 (.in0(in_6), .in1(1'b0), .out(multiplexer_5_out), .sel(PCLK));  // open: en
  Multiplexer multiplexer_6 (.in0(in_7), .in1(1'b0), .out(multiplexer_6_out), .sel(PCLK));  // open: en
  Multiplexer multiplexer_7 (.in0(in_8), .in1(1'b0), .out(multiplexer_7_out), .sel(PCLK));  // open: en
  Multiplexer multiplexer_8 (.in0(in_41), .in1(1'b1), .out(multiplexer_8_out), .sel(PCLK));  // open: en
  assign controlled_buffer_1_out = multiplexer_1_out ? multiplexer_8_out : 1'bz;  // Controlled_Buffer controlled_buffer_1
  assign controlled_buffer_2_out = multiplexer_1_out ? oam_cell_1_nout : 1'bz;  // Controlled_Buffer controlled_buffer_2
  assign controlled_buffer_3_out = multiplexer_2_out ? multiplexer_8_out : 1'bz;  // Controlled_Buffer controlled_buffer_3
  assign controlled_buffer_2_out = multiplexer_2_out ? oam_cell_3_nout : 1'bz;  // Controlled_Buffer controlled_buffer_4
  assign controlled_buffer_5_out = multiplexer_3_out ? multiplexer_8_out : 1'bz;  // Controlled_Buffer controlled_buffer_5
  assign controlled_buffer_2_out = multiplexer_3_out ? oam_cell_5_nout : 1'bz;  // Controlled_Buffer controlled_buffer_6
  assign controlled_buffer_7_out = multiplexer_4_out ? multiplexer_8_out : 1'bz;  // Controlled_Buffer controlled_buffer_7
  assign controlled_buffer_2_out = multiplexer_4_out ? oam_cell_7_nout : 1'bz;  // Controlled_Buffer controlled_buffer_8
  assign controlled_buffer_9_out = multiplexer_5_out ? multiplexer_8_out : 1'bz;  // Controlled_Buffer controlled_buffer_9
  assign controlled_buffer_2_out = multiplexer_5_out ? oam_cell_9_nout : 1'bz;  // Controlled_Buffer controlled_buffer_10
  assign controlled_buffer_11_out = multiplexer_6_out ? multiplexer_8_out : 1'bz;  // Controlled_Buffer controlled_buffer_11
  assign controlled_buffer_2_out = multiplexer_6_out ? oam_cell_11_nout : 1'bz;  // Controlled_Buffer controlled_buffer_12
  assign controlled_buffer_13_out = multiplexer_7_out ? multiplexer_8_out : 1'bz;  // Controlled_Buffer controlled_buffer_13
  assign controlled_buffer_2_out = multiplexer_7_out ? oam_cell_13_nout : 1'bz;  // Controlled_Buffer controlled_buffer_14
  Multiplexer multiplexer_9 (.in0(controlled_buffer_2_out), .in1(1'b1), .out(out_42), .sel(PCLK));  // open: en
  OAM_CELL oam_cell_1 (.enable(in_9), .in(controlled_buffer_1_out), .nout(oam_cell_1_nout));
  OAM_CELL oam_cell_2 (.enable(in_10), .in(controlled_buffer_1_out), .nout(oam_cell_1_nout));
  OAM_CELL oam_cell_3 (.enable(in_9), .in(controlled_buffer_3_out), .nout(oam_cell_3_nout));
  OAM_CELL oam_cell_4 (.enable(in_10), .in(controlled_buffer_3_out), .nout(oam_cell_3_nout));
  OAM_CELL oam_cell_5 (.enable(in_10), .in(controlled_buffer_5_out), .nout(oam_cell_5_nout));
  OAM_CELL oam_cell_6 (.enable(in_9), .in(controlled_buffer_5_out), .nout(oam_cell_5_nout));
  OAM_CELL oam_cell_7 (.enable(in_9), .in(controlled_buffer_7_out), .nout(oam_cell_7_nout));
  OAM_CELL oam_cell_8 (.enable(in_10), .in(controlled_buffer_7_out), .nout(oam_cell_7_nout));
  OAM_CELL oam_cell_9 (.enable(in_9), .in(controlled_buffer_9_out), .nout(oam_cell_9_nout));
  OAM_CELL oam_cell_10 (.enable(in_10), .in(controlled_buffer_9_out), .nout(oam_cell_9_nout));
  OAM_CELL oam_cell_11 (.enable(in_9), .in(controlled_buffer_11_out), .nout(oam_cell_11_nout));
  OAM_CELL oam_cell_12 (.enable(in_10), .in(controlled_buffer_11_out), .nout(oam_cell_11_nout));
  OAM_CELL oam_cell_13 (.enable(in_9), .in(controlled_buffer_13_out), .nout(oam_cell_13_nout));
  OAM_CELL oam_cell_14 (.enable(in_10), .in(controlled_buffer_13_out), .nout(oam_cell_13_nout));
  OAM_CELL oam_cell_15 (.enable(in_11), .in(controlled_buffer_1_out), .nout(oam_cell_1_nout));
  OAM_CELL oam_cell_16 (.enable(in_11), .in(controlled_buffer_3_out), .nout(oam_cell_3_nout));
  OAM_CELL oam_cell_17 (.enable(in_11), .in(controlled_buffer_5_out), .nout(oam_cell_5_nout));
  OAM_CELL oam_cell_18 (.enable(in_11), .in(controlled_buffer_7_out), .nout(oam_cell_7_nout));
  OAM_CELL oam_cell_19 (.enable(in_11), .in(controlled_buffer_9_out), .nout(oam_cell_9_nout));
  OAM_CELL oam_cell_20 (.enable(in_11), .in(controlled_buffer_11_out), .nout(oam_cell_11_nout));
  OAM_CELL oam_cell_21 (.enable(in_11), .in(controlled_buffer_13_out), .nout(oam_cell_13_nout));
  OAM_CELL oam_cell_22 (.enable(in_12), .in(controlled_buffer_1_out), .nout(oam_cell_1_nout));
  OAM_CELL oam_cell_23 (.enable(in_12), .in(controlled_buffer_3_out), .nout(oam_cell_3_nout));
  OAM_CELL oam_cell_24 (.enable(in_12), .in(controlled_buffer_5_out), .nout(oam_cell_5_nout));
  OAM_CELL oam_cell_25 (.enable(in_12), .in(controlled_buffer_7_out), .nout(oam_cell_7_nout));
  OAM_CELL oam_cell_26 (.enable(in_12), .in(controlled_buffer_9_out), .nout(oam_cell_9_nout));
  OAM_CELL oam_cell_27 (.enable(in_12), .in(controlled_buffer_11_out), .nout(oam_cell_11_nout));
  OAM_CELL oam_cell_28 (.enable(in_12), .in(controlled_buffer_13_out), .nout(oam_cell_13_nout));
  OAM_CELL oam_cell_29 (.enable(in_13), .in(controlled_buffer_1_out), .nout(oam_cell_1_nout));
  OAM_CELL oam_cell_30 (.enable(in_13), .in(controlled_buffer_3_out), .nout(oam_cell_3_nout));
  OAM_CELL oam_cell_31 (.enable(in_13), .in(controlled_buffer_5_out), .nout(oam_cell_5_nout));
  OAM_CELL oam_cell_32 (.enable(in_13), .in(controlled_buffer_7_out), .nout(oam_cell_7_nout));
  OAM_CELL oam_cell_33 (.enable(in_13), .in(controlled_buffer_9_out), .nout(oam_cell_9_nout));
  OAM_CELL oam_cell_34 (.enable(in_13), .in(controlled_buffer_11_out), .nout(oam_cell_11_nout));
  OAM_CELL oam_cell_35 (.enable(in_13), .in(controlled_buffer_13_out), .nout(oam_cell_13_nout));
  OAM_CELL oam_cell_36 (.enable(in_14), .in(controlled_buffer_1_out), .nout(oam_cell_1_nout));
  OAM_CELL oam_cell_37 (.enable(in_14), .in(controlled_buffer_3_out), .nout(oam_cell_3_nout));
  OAM_CELL oam_cell_38 (.enable(in_14), .in(controlled_buffer_5_out), .nout(oam_cell_5_nout));
  OAM_CELL oam_cell_39 (.enable(in_14), .in(controlled_buffer_7_out), .nout(oam_cell_7_nout));
  OAM_CELL oam_cell_40 (.enable(in_14), .in(controlled_buffer_9_out), .nout(oam_cell_9_nout));
  OAM_CELL oam_cell_41 (.enable(in_14), .in(controlled_buffer_11_out), .nout(oam_cell_11_nout));
  OAM_CELL oam_cell_42 (.enable(in_14), .in(controlled_buffer_13_out), .nout(oam_cell_13_nout));
  OAM_CELL oam_cell_43 (.enable(in_15), .in(controlled_buffer_1_out), .nout(oam_cell_1_nout));
  OAM_CELL oam_cell_44 (.enable(in_15), .in(controlled_buffer_3_out), .nout(oam_cell_3_nout));
  OAM_CELL oam_cell_45 (.enable(in_15), .in(controlled_buffer_5_out), .nout(oam_cell_5_nout));
  OAM_CELL oam_cell_46 (.enable(in_15), .in(controlled_buffer_7_out), .nout(oam_cell_7_nout));
  OAM_CELL oam_cell_47 (.enable(in_15), .in(controlled_buffer_9_out), .nout(oam_cell_9_nout));
  OAM_CELL oam_cell_48 (.enable(in_15), .in(controlled_buffer_11_out), .nout(oam_cell_11_nout));
  OAM_CELL oam_cell_49 (.enable(in_15), .in(controlled_buffer_13_out), .nout(oam_cell_13_nout));
  OAM_CELL oam_cell_50 (.enable(in_16), .in(controlled_buffer_1_out), .nout(oam_cell_1_nout));
  OAM_CELL oam_cell_51 (.enable(in_16), .in(controlled_buffer_3_out), .nout(oam_cell_3_nout));
  OAM_CELL oam_cell_52 (.enable(in_16), .in(controlled_buffer_5_out), .nout(oam_cell_5_nout));
  OAM_CELL oam_cell_53 (.enable(in_16), .in(controlled_buffer_7_out), .nout(oam_cell_7_nout));
  OAM_CELL oam_cell_54 (.enable(in_16), .in(controlled_buffer_9_out), .nout(oam_cell_9_nout));
  OAM_CELL oam_cell_55 (.enable(in_16), .in(controlled_buffer_11_out), .nout(oam_cell_11_nout));
  OAM_CELL oam_cell_56 (.enable(in_16), .in(controlled_buffer_13_out), .nout(oam_cell_13_nout));
  OAM_CELL oam_cell_57 (.enable(in_18), .in(controlled_buffer_1_out), .nout(oam_cell_1_nout));
  OAM_CELL oam_cell_58 (.enable(in_17), .in(controlled_buffer_1_out), .nout(oam_cell_1_nout));
  OAM_CELL oam_cell_59 (.enable(in_17), .in(controlled_buffer_3_out), .nout(oam_cell_3_nout));
  OAM_CELL oam_cell_60 (.enable(in_18), .in(controlled_buffer_3_out), .nout(oam_cell_3_nout));
  OAM_CELL oam_cell_61 (.enable(in_17), .in(controlled_buffer_5_out), .nout(oam_cell_5_nout));
  OAM_CELL oam_cell_62 (.enable(in_18), .in(controlled_buffer_5_out), .nout(oam_cell_5_nout));
  OAM_CELL oam_cell_63 (.enable(in_17), .in(controlled_buffer_7_out), .nout(oam_cell_7_nout));
  OAM_CELL oam_cell_64 (.enable(in_18), .in(controlled_buffer_7_out), .nout(oam_cell_7_nout));
  OAM_CELL oam_cell_65 (.enable(in_18), .in(controlled_buffer_9_out), .nout(oam_cell_9_nout));
  OAM_CELL oam_cell_66 (.enable(in_17), .in(controlled_buffer_9_out), .nout(oam_cell_9_nout));
  OAM_CELL oam_cell_67 (.enable(in_17), .in(controlled_buffer_11_out), .nout(oam_cell_11_nout));
  OAM_CELL oam_cell_68 (.enable(in_18), .in(controlled_buffer_11_out), .nout(oam_cell_11_nout));
  OAM_CELL oam_cell_69 (.enable(in_17), .in(controlled_buffer_13_out), .nout(oam_cell_13_nout));
  OAM_CELL oam_cell_70 (.enable(in_18), .in(controlled_buffer_13_out), .nout(oam_cell_13_nout));
  OAM_CELL oam_cell_71 (.enable(in_19), .in(controlled_buffer_1_out), .nout(oam_cell_1_nout));
  OAM_CELL oam_cell_72 (.enable(in_19), .in(controlled_buffer_3_out), .nout(oam_cell_3_nout));
  OAM_CELL oam_cell_73 (.enable(in_19), .in(controlled_buffer_5_out), .nout(oam_cell_5_nout));
  OAM_CELL oam_cell_74 (.enable(in_19), .in(controlled_buffer_7_out), .nout(oam_cell_7_nout));
  OAM_CELL oam_cell_75 (.enable(in_19), .in(controlled_buffer_9_out), .nout(oam_cell_9_nout));
  OAM_CELL oam_cell_76 (.enable(in_19), .in(controlled_buffer_11_out), .nout(oam_cell_11_nout));
  OAM_CELL oam_cell_77 (.enable(in_19), .in(controlled_buffer_13_out), .nout(oam_cell_13_nout));
  OAM_CELL oam_cell_78 (.enable(in_20), .in(controlled_buffer_1_out), .nout(oam_cell_1_nout));
  OAM_CELL oam_cell_79 (.enable(in_20), .in(controlled_buffer_3_out), .nout(oam_cell_3_nout));
  OAM_CELL oam_cell_80 (.enable(in_20), .in(controlled_buffer_5_out), .nout(oam_cell_5_nout));
  OAM_CELL oam_cell_81 (.enable(in_20), .in(controlled_buffer_7_out), .nout(oam_cell_7_nout));
  OAM_CELL oam_cell_82 (.enable(in_20), .in(controlled_buffer_9_out), .nout(oam_cell_9_nout));
  OAM_CELL oam_cell_83 (.enable(in_20), .in(controlled_buffer_11_out), .nout(oam_cell_11_nout));
  OAM_CELL oam_cell_84 (.enable(in_20), .in(controlled_buffer_13_out), .nout(oam_cell_13_nout));
  OAM_CELL oam_cell_85 (.enable(in_21), .in(controlled_buffer_1_out), .nout(oam_cell_1_nout));
  OAM_CELL oam_cell_86 (.enable(in_21), .in(controlled_buffer_3_out), .nout(oam_cell_3_nout));
  OAM_CELL oam_cell_87 (.enable(in_21), .in(controlled_buffer_5_out), .nout(oam_cell_5_nout));
  OAM_CELL oam_cell_88 (.enable(in_21), .in(controlled_buffer_7_out), .nout(oam_cell_7_nout));
  OAM_CELL oam_cell_89 (.enable(in_21), .in(controlled_buffer_9_out), .nout(oam_cell_9_nout));
  OAM_CELL oam_cell_90 (.enable(in_21), .in(controlled_buffer_11_out), .nout(oam_cell_11_nout));
  OAM_CELL oam_cell_91 (.enable(in_21), .in(controlled_buffer_13_out), .nout(oam_cell_13_nout));
  OAM_CELL oam_cell_92 (.enable(in_22), .in(controlled_buffer_1_out), .nout(oam_cell_1_nout));
  OAM_CELL oam_cell_93 (.enable(in_22), .in(controlled_buffer_3_out), .nout(oam_cell_3_nout));
  OAM_CELL oam_cell_94 (.enable(in_22), .in(controlled_buffer_5_out), .nout(oam_cell_5_nout));
  OAM_CELL oam_cell_95 (.enable(in_22), .in(controlled_buffer_7_out), .nout(oam_cell_7_nout));
  OAM_CELL oam_cell_96 (.enable(in_22), .in(controlled_buffer_9_out), .nout(oam_cell_9_nout));
  OAM_CELL oam_cell_97 (.enable(in_22), .in(controlled_buffer_11_out), .nout(oam_cell_11_nout));
  OAM_CELL oam_cell_98 (.enable(in_22), .in(controlled_buffer_13_out), .nout(oam_cell_13_nout));
  OAM_CELL oam_cell_99 (.enable(in_23), .in(controlled_buffer_1_out), .nout(oam_cell_1_nout));
  OAM_CELL oam_cell_100 (.enable(in_23), .in(controlled_buffer_3_out), .nout(oam_cell_3_nout));
  OAM_CELL oam_cell_101 (.enable(in_23), .in(controlled_buffer_5_out), .nout(oam_cell_5_nout));
  OAM_CELL oam_cell_102 (.enable(in_23), .in(controlled_buffer_7_out), .nout(oam_cell_7_nout));
  OAM_CELL oam_cell_103 (.enable(in_23), .in(controlled_buffer_9_out), .nout(oam_cell_9_nout));
  OAM_CELL oam_cell_104 (.enable(in_23), .in(controlled_buffer_11_out), .nout(oam_cell_11_nout));
  OAM_CELL oam_cell_105 (.enable(in_23), .in(controlled_buffer_13_out), .nout(oam_cell_13_nout));
  OAM_CELL oam_cell_106 (.enable(in_24), .in(controlled_buffer_1_out), .nout(oam_cell_1_nout));
  OAM_CELL oam_cell_107 (.enable(in_24), .in(controlled_buffer_3_out), .nout(oam_cell_3_nout));
  OAM_CELL oam_cell_108 (.enable(in_24), .in(controlled_buffer_5_out), .nout(oam_cell_5_nout));
  OAM_CELL oam_cell_109 (.enable(in_24), .in(controlled_buffer_7_out), .nout(oam_cell_7_nout));
  OAM_CELL oam_cell_110 (.enable(in_24), .in(controlled_buffer_9_out), .nout(oam_cell_9_nout));
  OAM_CELL oam_cell_111 (.enable(in_24), .in(controlled_buffer_11_out), .nout(oam_cell_11_nout));
  OAM_CELL oam_cell_112 (.enable(in_24), .in(controlled_buffer_13_out), .nout(oam_cell_13_nout));
  OAM_CELL oam_cell_113 (.enable(in_26), .in(controlled_buffer_1_out), .nout(oam_cell_1_nout));
  OAM_CELL oam_cell_114 (.enable(in_25), .in(controlled_buffer_1_out), .nout(oam_cell_1_nout));
  OAM_CELL oam_cell_115 (.enable(in_26), .in(controlled_buffer_3_out), .nout(oam_cell_3_nout));
  OAM_CELL oam_cell_116 (.enable(in_25), .in(controlled_buffer_3_out), .nout(oam_cell_3_nout));
  OAM_CELL oam_cell_117 (.enable(in_26), .in(controlled_buffer_5_out), .nout(oam_cell_5_nout));
  OAM_CELL oam_cell_118 (.enable(in_25), .in(controlled_buffer_5_out), .nout(oam_cell_5_nout));
  OAM_CELL oam_cell_119 (.enable(in_26), .in(controlled_buffer_7_out), .nout(oam_cell_7_nout));
  OAM_CELL oam_cell_120 (.enable(in_25), .in(controlled_buffer_7_out), .nout(oam_cell_7_nout));
  OAM_CELL oam_cell_121 (.enable(in_25), .in(controlled_buffer_9_out), .nout(oam_cell_9_nout));
  OAM_CELL oam_cell_122 (.enable(in_26), .in(controlled_buffer_9_out), .nout(oam_cell_9_nout));
  OAM_CELL oam_cell_123 (.enable(in_25), .in(controlled_buffer_11_out), .nout(oam_cell_11_nout));
  OAM_CELL oam_cell_124 (.enable(in_26), .in(controlled_buffer_11_out), .nout(oam_cell_11_nout));
  OAM_CELL oam_cell_125 (.enable(in_25), .in(controlled_buffer_13_out), .nout(oam_cell_13_nout));
  OAM_CELL oam_cell_126 (.enable(in_26), .in(controlled_buffer_13_out), .nout(oam_cell_13_nout));
  OAM_CELL oam_cell_127 (.enable(in_27), .in(controlled_buffer_1_out), .nout(oam_cell_1_nout));
  OAM_CELL oam_cell_128 (.enable(in_27), .in(controlled_buffer_3_out), .nout(oam_cell_3_nout));
  OAM_CELL oam_cell_129 (.enable(in_27), .in(controlled_buffer_5_out), .nout(oam_cell_5_nout));
  OAM_CELL oam_cell_130 (.enable(in_27), .in(controlled_buffer_7_out), .nout(oam_cell_7_nout));
  OAM_CELL oam_cell_131 (.enable(in_27), .in(controlled_buffer_9_out), .nout(oam_cell_9_nout));
  OAM_CELL oam_cell_132 (.enable(in_27), .in(controlled_buffer_11_out), .nout(oam_cell_11_nout));
  OAM_CELL oam_cell_133 (.enable(in_27), .in(controlled_buffer_13_out), .nout(oam_cell_13_nout));
  OAM_CELL oam_cell_134 (.enable(in_28), .in(controlled_buffer_1_out), .nout(oam_cell_1_nout));
  OAM_CELL oam_cell_135 (.enable(in_28), .in(controlled_buffer_3_out), .nout(oam_cell_3_nout));
  OAM_CELL oam_cell_136 (.enable(in_28), .in(controlled_buffer_5_out), .nout(oam_cell_5_nout));
  OAM_CELL oam_cell_137 (.enable(in_28), .in(controlled_buffer_7_out), .nout(oam_cell_7_nout));
  OAM_CELL oam_cell_138 (.enable(in_28), .in(controlled_buffer_9_out), .nout(oam_cell_9_nout));
  OAM_CELL oam_cell_139 (.enable(in_28), .in(controlled_buffer_11_out), .nout(oam_cell_11_nout));
  OAM_CELL oam_cell_140 (.enable(in_28), .in(controlled_buffer_13_out), .nout(oam_cell_13_nout));
  OAM_CELL oam_cell_141 (.enable(in_29), .in(controlled_buffer_1_out), .nout(oam_cell_1_nout));
  OAM_CELL oam_cell_142 (.enable(in_29), .in(controlled_buffer_3_out), .nout(oam_cell_3_nout));
  OAM_CELL oam_cell_143 (.enable(in_29), .in(controlled_buffer_5_out), .nout(oam_cell_5_nout));
  OAM_CELL oam_cell_144 (.enable(in_29), .in(controlled_buffer_7_out), .nout(oam_cell_7_nout));
  OAM_CELL oam_cell_145 (.enable(in_29), .in(controlled_buffer_9_out), .nout(oam_cell_9_nout));
  OAM_CELL oam_cell_146 (.enable(in_29), .in(controlled_buffer_11_out), .nout(oam_cell_11_nout));
  OAM_CELL oam_cell_147 (.enable(in_29), .in(controlled_buffer_13_out), .nout(oam_cell_13_nout));
  OAM_CELL oam_cell_148 (.enable(in_30), .in(controlled_buffer_1_out), .nout(oam_cell_1_nout));
  OAM_CELL oam_cell_149 (.enable(in_30), .in(controlled_buffer_3_out), .nout(oam_cell_3_nout));
  OAM_CELL oam_cell_150 (.enable(in_30), .in(controlled_buffer_5_out), .nout(oam_cell_5_nout));
  OAM_CELL oam_cell_151 (.enable(in_30), .in(controlled_buffer_7_out), .nout(oam_cell_7_nout));
  OAM_CELL oam_cell_152 (.enable(in_30), .in(controlled_buffer_9_out), .nout(oam_cell_9_nout));
  OAM_CELL oam_cell_153 (.enable(in_30), .in(controlled_buffer_11_out), .nout(oam_cell_11_nout));
  OAM_CELL oam_cell_154 (.enable(in_30), .in(controlled_buffer_13_out), .nout(oam_cell_13_nout));
  OAM_CELL oam_cell_155 (.enable(in_31), .in(controlled_buffer_1_out), .nout(oam_cell_1_nout));
  OAM_CELL oam_cell_156 (.enable(in_31), .in(controlled_buffer_3_out), .nout(oam_cell_3_nout));
  OAM_CELL oam_cell_157 (.enable(in_31), .in(controlled_buffer_5_out), .nout(oam_cell_5_nout));
  OAM_CELL oam_cell_158 (.enable(in_31), .in(controlled_buffer_7_out), .nout(oam_cell_7_nout));
  OAM_CELL oam_cell_159 (.enable(in_31), .in(controlled_buffer_9_out), .nout(oam_cell_9_nout));
  OAM_CELL oam_cell_160 (.enable(in_31), .in(controlled_buffer_11_out), .nout(oam_cell_11_nout));
  OAM_CELL oam_cell_161 (.enable(in_31), .in(controlled_buffer_13_out), .nout(oam_cell_13_nout));
  OAM_CELL oam_cell_162 (.enable(in_32), .in(controlled_buffer_1_out), .nout(oam_cell_1_nout));
  OAM_CELL oam_cell_163 (.enable(in_32), .in(controlled_buffer_3_out), .nout(oam_cell_3_nout));
  OAM_CELL oam_cell_164 (.enable(in_32), .in(controlled_buffer_5_out), .nout(oam_cell_5_nout));
  OAM_CELL oam_cell_165 (.enable(in_32), .in(controlled_buffer_7_out), .nout(oam_cell_7_nout));
  OAM_CELL oam_cell_166 (.enable(in_32), .in(controlled_buffer_9_out), .nout(oam_cell_9_nout));
  OAM_CELL oam_cell_167 (.enable(in_32), .in(controlled_buffer_11_out), .nout(oam_cell_11_nout));
  OAM_CELL oam_cell_168 (.enable(in_32), .in(controlled_buffer_13_out), .nout(oam_cell_13_nout));
  OAM_CELL oam_cell_169 (.enable(in_33), .in(controlled_buffer_1_out), .nout(oam_cell_1_nout));
  OAM_CELL oam_cell_170 (.enable(in_34), .in(controlled_buffer_1_out), .nout(oam_cell_1_nout));
  OAM_CELL oam_cell_171 (.enable(in_33), .in(controlled_buffer_3_out), .nout(oam_cell_3_nout));
  OAM_CELL oam_cell_172 (.enable(in_34), .in(controlled_buffer_3_out), .nout(oam_cell_3_nout));
  OAM_CELL oam_cell_173 (.enable(in_33), .in(controlled_buffer_5_out), .nout(oam_cell_5_nout));
  OAM_CELL oam_cell_174 (.enable(in_34), .in(controlled_buffer_5_out), .nout(oam_cell_5_nout));
  OAM_CELL oam_cell_175 (.enable(in_34), .in(controlled_buffer_7_out), .nout(oam_cell_7_nout));
  OAM_CELL oam_cell_176 (.enable(in_33), .in(controlled_buffer_7_out), .nout(oam_cell_7_nout));
  OAM_CELL oam_cell_177 (.enable(in_34), .in(controlled_buffer_9_out), .nout(oam_cell_9_nout));
  OAM_CELL oam_cell_178 (.enable(in_33), .in(controlled_buffer_9_out), .nout(oam_cell_9_nout));
  OAM_CELL oam_cell_179 (.enable(in_33), .in(controlled_buffer_11_out), .nout(oam_cell_11_nout));
  OAM_CELL oam_cell_180 (.enable(in_34), .in(controlled_buffer_11_out), .nout(oam_cell_11_nout));
  OAM_CELL oam_cell_181 (.enable(in_33), .in(controlled_buffer_13_out), .nout(oam_cell_13_nout));
  OAM_CELL oam_cell_182 (.enable(in_34), .in(controlled_buffer_13_out), .nout(oam_cell_13_nout));
  OAM_CELL oam_cell_183 (.enable(in_35), .in(controlled_buffer_1_out), .nout(oam_cell_1_nout));
  OAM_CELL oam_cell_184 (.enable(in_35), .in(controlled_buffer_3_out), .nout(oam_cell_3_nout));
  OAM_CELL oam_cell_185 (.enable(in_35), .in(controlled_buffer_5_out), .nout(oam_cell_5_nout));
  OAM_CELL oam_cell_186 (.enable(in_35), .in(controlled_buffer_7_out), .nout(oam_cell_7_nout));
  OAM_CELL oam_cell_187 (.enable(in_35), .in(controlled_buffer_9_out), .nout(oam_cell_9_nout));
  OAM_CELL oam_cell_188 (.enable(in_35), .in(controlled_buffer_11_out), .nout(oam_cell_11_nout));
  OAM_CELL oam_cell_189 (.enable(in_35), .in(controlled_buffer_13_out), .nout(oam_cell_13_nout));
  OAM_CELL oam_cell_190 (.enable(in_36), .in(controlled_buffer_1_out), .nout(oam_cell_1_nout));
  OAM_CELL oam_cell_191 (.enable(in_36), .in(controlled_buffer_3_out), .nout(oam_cell_3_nout));
  OAM_CELL oam_cell_192 (.enable(in_36), .in(controlled_buffer_5_out), .nout(oam_cell_5_nout));
  OAM_CELL oam_cell_193 (.enable(in_36), .in(controlled_buffer_7_out), .nout(oam_cell_7_nout));
  OAM_CELL oam_cell_194 (.enable(in_36), .in(controlled_buffer_9_out), .nout(oam_cell_9_nout));
  OAM_CELL oam_cell_195 (.enable(in_36), .in(controlled_buffer_11_out), .nout(oam_cell_11_nout));
  OAM_CELL oam_cell_196 (.enable(in_36), .in(controlled_buffer_13_out), .nout(oam_cell_13_nout));
  OAM_CELL oam_cell_197 (.enable(in_37), .in(controlled_buffer_1_out), .nout(oam_cell_1_nout));
  OAM_CELL oam_cell_198 (.enable(in_37), .in(controlled_buffer_3_out), .nout(oam_cell_3_nout));
  OAM_CELL oam_cell_199 (.enable(in_37), .in(controlled_buffer_5_out), .nout(oam_cell_5_nout));
  OAM_CELL oam_cell_200 (.enable(in_37), .in(controlled_buffer_7_out), .nout(oam_cell_7_nout));
  OAM_CELL oam_cell_201 (.enable(in_37), .in(controlled_buffer_9_out), .nout(oam_cell_9_nout));
  OAM_CELL oam_cell_202 (.enable(in_37), .in(controlled_buffer_11_out), .nout(oam_cell_11_nout));
  OAM_CELL oam_cell_203 (.enable(in_37), .in(controlled_buffer_13_out), .nout(oam_cell_13_nout));
  OAM_CELL oam_cell_204 (.enable(in_38), .in(controlled_buffer_1_out), .nout(oam_cell_1_nout));
  OAM_CELL oam_cell_205 (.enable(in_38), .in(controlled_buffer_3_out), .nout(oam_cell_3_nout));
  OAM_CELL oam_cell_206 (.enable(in_38), .in(controlled_buffer_5_out), .nout(oam_cell_5_nout));
  OAM_CELL oam_cell_207 (.enable(in_38), .in(controlled_buffer_7_out), .nout(oam_cell_7_nout));
  OAM_CELL oam_cell_208 (.enable(in_38), .in(controlled_buffer_9_out), .nout(oam_cell_9_nout));
  OAM_CELL oam_cell_209 (.enable(in_38), .in(controlled_buffer_11_out), .nout(oam_cell_11_nout));
  OAM_CELL oam_cell_210 (.enable(in_38), .in(controlled_buffer_13_out), .nout(oam_cell_13_nout));
  OAM_CELL oam_cell_211 (.enable(in_39), .in(controlled_buffer_1_out), .nout(oam_cell_1_nout));
  OAM_CELL oam_cell_212 (.enable(in_39), .in(controlled_buffer_3_out), .nout(oam_cell_3_nout));
  OAM_CELL oam_cell_213 (.enable(in_39), .in(controlled_buffer_5_out), .nout(oam_cell_5_nout));
  OAM_CELL oam_cell_214 (.enable(in_39), .in(controlled_buffer_7_out), .nout(oam_cell_7_nout));
  OAM_CELL oam_cell_215 (.enable(in_39), .in(controlled_buffer_9_out), .nout(oam_cell_9_nout));
  OAM_CELL oam_cell_216 (.enable(in_39), .in(controlled_buffer_11_out), .nout(oam_cell_11_nout));
  OAM_CELL oam_cell_217 (.enable(in_39), .in(controlled_buffer_13_out), .nout(oam_cell_13_nout));
  OAM_CELL oam_cell_218 (.enable(in_40), .in(controlled_buffer_1_out), .nout(oam_cell_1_nout));
  OAM_CELL oam_cell_219 (.enable(in_40), .in(controlled_buffer_3_out), .nout(oam_cell_3_nout));
  OAM_CELL oam_cell_220 (.enable(in_40), .in(controlled_buffer_5_out), .nout(oam_cell_5_nout));
  OAM_CELL oam_cell_221 (.enable(in_40), .in(controlled_buffer_7_out), .nout(oam_cell_7_nout));
  OAM_CELL oam_cell_222 (.enable(in_40), .in(controlled_buffer_9_out), .nout(oam_cell_9_nout));
  OAM_CELL oam_cell_223 (.enable(in_40), .in(controlled_buffer_11_out), .nout(oam_cell_11_nout));
  OAM_CELL oam_cell_224 (.enable(in_40), .in(controlled_buffer_13_out), .nout(oam_cell_13_nout));
endmodule

// OAM BUF BIT
module OAM_BUFFER_BIT (
  input  PCLK,
  input  nR4,
  input  IOAM2,
  input  DB___OB,
  input  DB_OB,
  input  nOE,
  output OB___DB,
  output OB,
  output OR,
  output OW
);

  wire _7_out, _8_out, _12_out, d_latch_1_not_q, multiplexer_1_out, multiplexer_2_out, not_2_out, not_3_out,
       not_4_out, not_5_out;

  nor _8 (_8_out, IOAM2, _7_out);
  Multiplexer #(.enable("false")) multiplexer_1 (.in0(_8_out), .in1(not_2_out), .out(multiplexer_1_out), .sel(PCLK));
  not not_1 (OB, multiplexer_1_out);
  not not_2 (not_2_out, OB);
  D_latch d_latch_1 (.EN(PCLK), .D(OB), .NOT_Q(d_latch_1_not_q));  // open: Q
  Multiplexer #(.enable("false")) multiplexer_2 (.in0(DB___OB), .in1(OB), .out(multiplexer_2_out), .sel(DB_OB));
  not not_3 (not_3_out, nR4);
  not not_4 (not_4_out, multiplexer_2_out);
  not not_5 (not_5_out, nOE);
  Multiplexer multiplexer_3 (.in0(1'b1), .in1(1'b0), .out(OB___DB), .sel(d_latch_1_not_q), .en(not_3_out));
  Multiplexer multiplexer_4 (.in0(1'b0), .in1(1'b1), .out(OR), .sel(not_4_out), .en(not_5_out));
  Multiplexer multiplexer_5 (.in0(1'b1), .in1(1'b0), .out(OW), .sel(not_4_out), .en(not_5_out));
  nor _12 (_12_out, OW, _7_out);
  nor _7 (_7_out, _12_out, OR);
  assign OR = PCLK ? 1'b1 : 1'bz;  // Controlled_Buffer controlled_buffer_1
  assign OW = PCLK ? 1'b1 : 1'bz;  // Controlled_Buffer controlled_buffer_2
  assign _7_out = PCLK ? _12_out : 1'bz;  // Controlled_Buffer controlled_buffer_3

  // Notes on the sheet:
  //   1
  //   1011
  //   9
  //   4
endmodule

module VRAM_BUS_CONTROL (
  input  PCLK,
  input  nR7,
  input  RES,
  input  nDBE,
  input  nW7,
  input  BLNK,
  input  H0_prime,
  input  nPA8,
  input  nPA9,
  input  nPA10,
  input  nPA11,
  input  nPA12,
  output TSTEP,
  output PD_RB,
  output DB_PAR,
  output nALE,
  output RD,
  output WR,
  output XRB,
  output TH_MUX
);

  wire and_1_out, d_latch_1_not_q, d_latch_2_not_q, d_latch_3_not_q, d_latch_4_not_q, d_latch_4_q,
       d_latch_5_not_q, d_latch_6_not_q, d_latch_7_not_q, d_latch_7_q, d_latch_8_not_q, d_latch_8_q,
       d_latch_9_q, d_latch_10_q, d_latch_11_q, multiplexer_1_out, multiplexer_2_out, nand_1_out, nor_1_out,
       nor_2_out, nor_4_out, nor_5_out, nor_7_out, nor_9_out, nor_10_out, nor_12_out, nor_14_out, not_1_out,
       not_2_out, not_4_out, not_6_out, not_7_out, not_8_out, not_9_out, not_10_out, pull_resistor_1_node,
       pull_resistor_2_node, s_r_ff_1_q, s_r_ff_2_q;

  not not_1 (not_1_out, RES);
  not not_2 (not_2_out, PCLK);
  nor nor_1 (nor_1_out, nR7, nDBE);
  nor nor_2 (nor_2_out, nDBE, nW7);
  D_latch d_latch_1 (.EN(PCLK), .D(BLNK), .NOT_Q(d_latch_1_not_q));  // open: Q
  S_R_Flip_Flop #(.trigger("high")) s_r_ff_1 (
    .S(d_latch_6_not_q), .clk(1'b1), .R(nor_1_out), .Q(s_r_ff_1_q));  // open: Qn, preset, reset, en
  S_R_Flip_Flop #(.trigger("high")) s_r_ff_2 (
    .S(d_latch_7_not_q), .clk(1'b1), .R(nor_2_out), .Q(s_r_ff_2_q));  // open: Qn, preset, reset, en
  nor nor_3 (TH_MUX, d_latch_1_not_q, nPA8, nPA9, nPA10, nPA11, nPA12);
  Pull_Resistor pull_resistor_1 (.node(pull_resistor_1_node));
  nor nor_4 (nor_4_out, s_r_ff_1_q, nor_1_out);
  Pull_Resistor pull_resistor_2 (.node(pull_resistor_2_node));
  nor nor_5 (nor_5_out, s_r_ff_2_q, nor_2_out);
  not not_3 (pull_resistor_1_node, not_4_out);
  Multiplexer multiplexer_1 (
    .in0(pull_resistor_1_node), .in1(nor_4_out), .out(multiplexer_1_out), .sel(PCLK), .en(not_1_out));
  not not_4 (not_4_out, multiplexer_1_out);
  not not_5 (pull_resistor_2_node, not_6_out);
  not not_6 (not_6_out, multiplexer_2_out);
  Multiplexer #(.disabled(0)) multiplexer_2 (
    .in0(pull_resistor_2_node), .in1(nor_5_out), .out(multiplexer_2_out), .sel(PCLK), .en(not_1_out));
  D_latch d_latch_2 (.EN(not_2_out), .D(not_4_out), .NOT_Q(d_latch_2_not_q));  // open: Q
  D_latch d_latch_3 (.EN(not_2_out), .D(not_6_out), .NOT_Q(d_latch_3_not_q));  // open: Q
  D_latch d_latch_4 (.EN(PCLK), .D(d_latch_2_not_q), .Q(d_latch_4_q), .NOT_Q(d_latch_4_not_q));
  D_latch d_latch_5 (.EN(PCLK), .D(d_latch_3_not_q), .NOT_Q(d_latch_5_not_q));  // open: Q
  D_latch d_latch_6 (.EN(not_2_out), .D(d_latch_4_not_q), .NOT_Q(d_latch_6_not_q));  // open: Q
  D_latch d_latch_7 (.EN(not_2_out), .D(d_latch_5_not_q), .Q(d_latch_7_q), .NOT_Q(d_latch_7_not_q));
  D_latch d_latch_8 (.EN(PCLK), .D(d_latch_6_not_q), .Q(d_latch_8_q), .NOT_Q(d_latch_8_not_q));
  D_latch d_latch_9 (.EN(PCLK), .D(d_latch_7_not_q), .Q(d_latch_9_q));  // open: NOT_Q
  D_latch d_latch_10 (.EN(PCLK), .D(H0_prime), .Q(d_latch_10_q));  // open: NOT_Q
  nor nor_6 (PD_RB, d_latch_4_q, d_latch_8_not_q);
  nor nor_7 (nor_7_out, d_latch_8_q, d_latch_4_not_q);
  nor nor_8 (DB_PAR, d_latch_3_not_q, d_latch_7_q);
  nor nor_9 (nor_9_out, d_latch_9_q, d_latch_5_not_q);
  nor nor_10 (nor_10_out, not_2_out, H0_prime, BLNK);
  not not_7 (not_7_out, BLNK);
  nor nor_11 (nALE, nor_7_out, nor_9_out, nor_10_out);
  nand nand_1 (nand_1_out, not_7_out, d_latch_10_q);
  D_latch d_latch_11 (.EN(PCLK), .D(DB_PAR), .Q(d_latch_11_q));  // open: NOT_Q
  nor nor_12 (nor_12_out, d_latch_11_q, PD_RB);
  not not_8 (not_8_out, PD_RB);
  and and_1 (and_1_out, not_8_out, nand_1_out);
  not not_9 (not_9_out, DB_PAR);
  nor nor_13 (WR, not_9_out, TH_MUX);
  not not_10 (not_10_out, nor_1_out);
  nor nor_14 (nor_14_out, not_10_out, TH_MUX);
  not not_11 (TSTEP, nor_12_out);
  not not_12 (RD, and_1_out);
  not not_13 (XRB, nor_14_out);

  // Notes on the sheet:
  //   W7_EN
  //   R7_EN
  //   /PCLK
  //   /PCLK
  //   PCLK
  //   PCLK
  //   /PCLK
  //   /PCLK
  //   H0'
  //   PCLK
  //   PCLK
  //   H0'
  //   BLNK
  //   H0''
  //   PD/RB
  //   DB/PAR
  //   /ALE
endmodule
// BG COLOR
module BG_COLOR (
  input  PCLK,
  input  CLPB,
  input  FH0,
  input  FH1,
  input  FH2,
  input  PD0,
  input  PD1,
  input  PD2,
  input  PD3,
  input  PD4,
  input  PD5,
  input  PD6,
  input  PD7,
  input  THO1,
  input  TVO1,
  input  F_AT,
  input  H0_prime_prime,
  input  F_TA,
  input  F_TB,
  input  nFO,
  output BGC0,
  output BGC1,
  output BGC2,
  output BGC3
);

  wire d_latch_9_q, d_latch_10_not_q, d_latch_11_not_q, d_latch_12_not_q, d_latch_13_not_q, d_latch_14_not_q,
       d_latch_15_not_q, d_latch_16_not_q, d_latch_17_not_q, d_latch_18_q, d_latch_19_not_q,
       d_latch_20_not_q, d_latch_21_not_q, d_latch_22_not_q, d_latch_23_not_q, d_latch_24_not_q,
       d_latch_25_not_q, d_latch_26_not_q, d_latch_27_not_q, d_latch_28_q, d_latch_29_q, d_latch_30_q,
       d_latch_31_q, nor_1_out, nor_2_out, nor_3_out, nor_4_out, nor_5_out, nor_6_out, nor_7_out, not_1_out,
       not_2_out, not_3_out, not_4_out, not_5_out, not_6_out, not_7_out, not_8_out, not_9_out, not_10_out,
       SEL_1_4_2_out, SEL_1_4_out, SEL_1_8_2_out, SEL_1_8_3_out, SEL_1_8_4_out, SEL_1_8_out,
       SHIFT_REGISTER_2_out_0, SHIFT_REGISTER_2_out_1, SHIFT_REGISTER_2_out_2, SHIFT_REGISTER_2_out_3,
       SHIFT_REGISTER_2_out_4, SHIFT_REGISTER_2_out_5, SHIFT_REGISTER_2_out_6, SHIFT_REGISTER_2_out_7,
       SHIFT_REGISTER_3_out_0, SHIFT_REGISTER_3_out_1, SHIFT_REGISTER_3_out_2, SHIFT_REGISTER_3_out_3,
       SHIFT_REGISTER_3_out_4, SHIFT_REGISTER_3_out_5, SHIFT_REGISTER_3_out_6, SHIFT_REGISTER_3_out_7,
       SHIFT_REGISTER_4_out_0, SHIFT_REGISTER_4_out_1, SHIFT_REGISTER_4_out_2, SHIFT_REGISTER_4_out_3,
       SHIFT_REGISTER_4_out_4, SHIFT_REGISTER_4_out_5, SHIFT_REGISTER_4_out_6, SHIFT_REGISTER_4_out_7,
       SHIFT_REGISTER_LOADABLE_2_out, SHIFT_REGISTER_LOADABLE_out, SHIFT_REGISTER_out_0,
       SHIFT_REGISTER_out_1, SHIFT_REGISTER_out_2, SHIFT_REGISTER_out_3, SHIFT_REGISTER_out_4,
       SHIFT_REGISTER_out_5, SHIFT_REGISTER_out_6, SHIFT_REGISTER_out_7;
  wire [7:0] d_latch_1_not_q;

  not not_1 (not_1_out, F_AT);
  not not_2 (not_2_out, H0_prime_prime);
  not not_3 (not_3_out, F_TA);
  not not_4 (not_4_out, F_TB);
  not not_5 (not_5_out, nFO);
  not not_6 (not_6_out, PCLK);
  nor nor_1 (nor_1_out, PCLK, d_latch_18_q, not_2_out);
  D_latch d_latch_1 (.EN(nor_2_out), .D(PD0), .NOT_Q(d_latch_1_not_q[0]));  // open: Q
  D_latch d_latch_2 (.EN(nor_2_out), .D(PD1), .NOT_Q(d_latch_1_not_q[1]));  // open: Q
  D_latch d_latch_3 (.EN(nor_2_out), .D(PD2), .NOT_Q(d_latch_1_not_q[2]));  // open: Q
  D_latch d_latch_4 (.EN(nor_2_out), .D(PD3), .NOT_Q(d_latch_1_not_q[3]));  // open: Q
  D_latch d_latch_5 (.EN(nor_2_out), .D(PD4), .NOT_Q(d_latch_1_not_q[4]));  // open: Q
  D_latch d_latch_6 (.EN(nor_2_out), .D(PD5), .NOT_Q(d_latch_1_not_q[5]));  // open: Q
  D_latch d_latch_7 (.EN(nor_2_out), .D(PD6), .NOT_Q(d_latch_1_not_q[6]));  // open: Q
  D_latch d_latch_8 (.EN(nor_2_out), .D(PD7), .NOT_Q(d_latch_1_not_q[7]));  // open: Q
  D_latch d_latch_9 (.EN(PCLK), .D(THO1), .Q(d_latch_9_q));  // open: NOT_Q
  D_latch d_latch_10 (.EN(nor_1_out), .D(PD1), .NOT_Q(d_latch_10_not_q));  // open: Q
  D_latch d_latch_11 (.EN(nor_1_out), .D(PD3), .NOT_Q(d_latch_11_not_q));  // open: Q
  D_latch d_latch_12 (.EN(nor_1_out), .D(PD5), .NOT_Q(d_latch_12_not_q));  // open: Q
  D_latch d_latch_13 (.EN(nor_1_out), .D(PD7), .NOT_Q(d_latch_13_not_q));  // open: Q
  D_latch d_latch_14 (.EN(nor_1_out), .D(PD0), .NOT_Q(d_latch_14_not_q));  // open: Q
  D_latch d_latch_15 (.EN(nor_1_out), .D(PD2), .NOT_Q(d_latch_15_not_q));  // open: Q
  D_latch d_latch_16 (.EN(nor_1_out), .D(PD4), .NOT_Q(d_latch_16_not_q));  // open: Q
  D_latch d_latch_17 (.EN(nor_1_out), .D(PD6), .NOT_Q(d_latch_17_not_q));  // open: Q
  D_latch d_latch_18 (.EN(PCLK), .D(not_1_out), .Q(d_latch_18_q));  // open: NOT_Q
  SEL_1_4 SEL_1_4 (
    .HO1(d_latch_9_q), .VO1(TVO1), ._0(d_latch_10_not_q), ._1(d_latch_11_not_q), ._2(d_latch_12_not_q),
    ._3(d_latch_13_not_q), .OUT(SEL_1_4_out));
  SEL_1_4 SEL_1_4_2 (
    .HO1(TVO1), .VO1(d_latch_9_q), ._0(d_latch_14_not_q), ._1(d_latch_15_not_q), ._2(d_latch_16_not_q),
    ._3(d_latch_17_not_q), .OUT(SEL_1_4_2_out));
  nor nor_2 (nor_2_out, PCLK, not_2_out, not_3_out);
  nor nor_3 (nor_3_out, PCLK, not_2_out, not_4_out);
  not not_7 (not_7_out, PCLK);
  D_latch d_latch_19 (.EN(nor_3_out), .D(SEL_1_4_out), .NOT_Q(d_latch_19_not_q));  // open: Q
  D_latch d_latch_20 (.EN(nor_3_out), .D(SEL_1_4_2_out), .NOT_Q(d_latch_20_not_q));  // open: Q
  nor nor_4 (nor_4_out, not_7_out, nor_5_out, nor_7_out);
  nor nor_5 (nor_5_out, PCLK, nor_6_out, not_5_out);
  nor nor_6 (nor_6_out, not_2_out, not_4_out);
  SHIFT_REG_LOAD SHIFT_REGISTER_LOADABLE (
    .LOAD(nor_3_out), .STEP(nor_5_out), .NEXT(nor_4_out), .OUT(SHIFT_REGISTER_LOADABLE_out),
    ._0(d_latch_1_not_q[0]), ._1(d_latch_1_not_q[1]), ._2(d_latch_1_not_q[2]), ._3(d_latch_1_not_q[3]),
    ._4(d_latch_1_not_q[4]), ._5(d_latch_1_not_q[5]), ._6(d_latch_1_not_q[6]), ._7(d_latch_1_not_q[7]));
  SHIFT_REG_LOAD SHIFT_REGISTER_LOADABLE_2 (
    .LOAD(nor_3_out), .STEP(nor_5_out), .NEXT(nor_4_out), .OUT(SHIFT_REGISTER_LOADABLE_2_out), ._0(PD0),
    ._1(PD1), ._2(PD2), ._3(PD3), ._4(PD4), ._5(PD5), ._6(PD6), ._7(PD7));
  D_latch d_latch_21 (.EN(nor_4_out), .D(d_latch_19_not_q), .NOT_Q(d_latch_21_not_q));  // open: Q
  D_latch d_latch_22 (.EN(nor_4_out), .D(d_latch_20_not_q), .NOT_Q(d_latch_22_not_q));  // open: Q
  nor nor_7 (nor_7_out, PCLK, not_5_out);
  SEL_1_8 SEL_1_8 (
    .FH0(FH0), .FH1(FH1), .FH2(FH2), .OUT(SEL_1_8_out), ._0(SHIFT_REGISTER_out_0), ._1(SHIFT_REGISTER_out_1),
    ._2(SHIFT_REGISTER_out_2), ._3(SHIFT_REGISTER_out_3), ._4(SHIFT_REGISTER_out_4),
    ._5(SHIFT_REGISTER_out_5), ._6(SHIFT_REGISTER_out_6), ._7(SHIFT_REGISTER_out_7));
  SHIFT_REG SHIFT_REGISTER (
    .STEP1(nor_7_out), .DATA_IN(SHIFT_REGISTER_LOADABLE_out), .STEP2(nor_4_out),
    .OUT_0(SHIFT_REGISTER_out_0), .OUT_1(SHIFT_REGISTER_out_1), .OUT_2(SHIFT_REGISTER_out_2),
    .OUT_3(SHIFT_REGISTER_out_3), .OUT_4(SHIFT_REGISTER_out_4), .OUT_5(SHIFT_REGISTER_out_5),
    .OUT_6(SHIFT_REGISTER_out_6), .OUT_7(SHIFT_REGISTER_out_7));
  SEL_1_8 SEL_1_8_2 (
    .FH0(FH0), .FH1(FH1), .FH2(FH2), .OUT(SEL_1_8_2_out), ._0(SHIFT_REGISTER_2_out_0),
    ._1(SHIFT_REGISTER_2_out_1), ._2(SHIFT_REGISTER_2_out_2), ._3(SHIFT_REGISTER_2_out_3),
    ._4(SHIFT_REGISTER_2_out_4), ._5(SHIFT_REGISTER_2_out_5), ._6(SHIFT_REGISTER_2_out_6),
    ._7(SHIFT_REGISTER_2_out_7));
  SHIFT_REG SHIFT_REGISTER_2 (
    .STEP1(nor_7_out), .DATA_IN(SHIFT_REGISTER_LOADABLE_2_out), .STEP2(nor_4_out),
    .OUT_0(SHIFT_REGISTER_2_out_0), .OUT_1(SHIFT_REGISTER_2_out_1), .OUT_2(SHIFT_REGISTER_2_out_2),
    .OUT_3(SHIFT_REGISTER_2_out_3), .OUT_4(SHIFT_REGISTER_2_out_4), .OUT_5(SHIFT_REGISTER_2_out_5),
    .OUT_6(SHIFT_REGISTER_2_out_6), .OUT_7(SHIFT_REGISTER_2_out_7));
  SEL_1_8 SEL_1_8_3 (
    .FH0(FH0), .FH1(FH1), .FH2(FH2), .OUT(SEL_1_8_3_out), ._0(SHIFT_REGISTER_3_out_0),
    ._1(SHIFT_REGISTER_3_out_1), ._2(SHIFT_REGISTER_3_out_2), ._3(SHIFT_REGISTER_3_out_3),
    ._4(SHIFT_REGISTER_3_out_4), ._5(SHIFT_REGISTER_3_out_5), ._6(SHIFT_REGISTER_3_out_6),
    ._7(SHIFT_REGISTER_3_out_7));
  SHIFT_REG SHIFT_REGISTER_3 (
    .STEP1(nor_7_out), .DATA_IN(d_latch_21_not_q), .STEP2(nor_4_out), .OUT_0(SHIFT_REGISTER_3_out_0),
    .OUT_1(SHIFT_REGISTER_3_out_1), .OUT_2(SHIFT_REGISTER_3_out_2), .OUT_3(SHIFT_REGISTER_3_out_3),
    .OUT_4(SHIFT_REGISTER_3_out_4), .OUT_5(SHIFT_REGISTER_3_out_5), .OUT_6(SHIFT_REGISTER_3_out_6),
    .OUT_7(SHIFT_REGISTER_3_out_7));
  SEL_1_8 SEL_1_8_4 (
    .FH0(FH0), .FH1(FH1), .FH2(FH2), .OUT(SEL_1_8_4_out), ._0(SHIFT_REGISTER_4_out_0),
    ._1(SHIFT_REGISTER_4_out_1), ._2(SHIFT_REGISTER_4_out_2), ._3(SHIFT_REGISTER_4_out_3),
    ._4(SHIFT_REGISTER_4_out_4), ._5(SHIFT_REGISTER_4_out_5), ._6(SHIFT_REGISTER_4_out_6),
    ._7(SHIFT_REGISTER_4_out_7));
  SHIFT_REG SHIFT_REGISTER_4 (
    .STEP1(nor_7_out), .DATA_IN(d_latch_22_not_q), .STEP2(nor_4_out), .OUT_0(SHIFT_REGISTER_4_out_0),
    .OUT_1(SHIFT_REGISTER_4_out_1), .OUT_2(SHIFT_REGISTER_4_out_2), .OUT_3(SHIFT_REGISTER_4_out_3),
    .OUT_4(SHIFT_REGISTER_4_out_4), .OUT_5(SHIFT_REGISTER_4_out_5), .OUT_6(SHIFT_REGISTER_4_out_6),
    .OUT_7(SHIFT_REGISTER_4_out_7));
  not not_8 (not_8_out, SEL_1_8_out);
  not not_9 (not_9_out, SEL_1_8_3_out);
  not not_10 (not_10_out, SEL_1_8_4_out);
  D_latch d_latch_23 (.EN(not_6_out), .D(not_8_out), .NOT_Q(d_latch_23_not_q));  // open: Q
  D_latch d_latch_24 (.EN(not_6_out), .D(SEL_1_8_2_out), .NOT_Q(d_latch_24_not_q));  // open: Q
  D_latch d_latch_25 (.EN(not_6_out), .D(not_9_out), .NOT_Q(d_latch_25_not_q));  // open: Q
  D_latch d_latch_26 (.EN(not_6_out), .D(not_10_out), .NOT_Q(d_latch_26_not_q));  // open: Q
  D_latch d_latch_27 (.EN(PCLK), .D(CLPB), .NOT_Q(d_latch_27_not_q));  // open: Q
  D_latch d_latch_28 (.EN(PCLK), .D(d_latch_23_not_q), .Q(d_latch_28_q));  // open: NOT_Q
  D_latch d_latch_29 (.EN(PCLK), .D(d_latch_24_not_q), .Q(d_latch_29_q));  // open: NOT_Q
  D_latch d_latch_30 (.EN(PCLK), .D(d_latch_25_not_q), .Q(d_latch_30_q));  // open: NOT_Q
  D_latch d_latch_31 (.EN(PCLK), .D(d_latch_26_not_q), .Q(d_latch_31_q));  // open: NOT_Q
  nor nor_8 (BGC0, d_latch_27_not_q, d_latch_28_q);
  nor nor_9 (BGC1, d_latch_27_not_q, d_latch_29_q);
  nor nor_10 (BGC2, d_latch_27_not_q, d_latch_30_q);
  nor nor_11 (BGC3, d_latch_27_not_q, d_latch_31_q);

  // Notes on the sheet:
  //   PD/SEL
  //   PD/SR
  //   STEP
  //   SRLOAD
  //   NEXT
  //   STEP2
  //   PCLK
  //   /PCLK
endmodule

module PICTURE_ADDRESS_GEN (
  input  PCLK,
  input  F_AT,
  input  F_NT,
  input  PAR_O,
  input  SH2,
  input  O8_16,
  input  OBSEL,
  input  BGSEL,
  input  H2_prime,
  input  H1_prime,
  input  SC_CNT,
  input  RESCL,
  input  E_EV,
  input  TSTEP,
  input  F_TB,
  input  H0_prime_prime,
  input  BLNK,
  input  l1_32,
  input  PD0,
  input  PD1,
  input  PD2,
  input  PD3,
  input  PD4,
  input  PD5,
  input  PD6,
  input  PD7,
  input  OB0,
  input  OB1,
  input  OB2,
  input  OB3,
  input  OB4,
  input  OB5,
  input  OB6,
  input  OB7,
  input  OV0,
  input  OV1,
  input  OV2,
  input  OV3,
  input  DB0,
  input  DB1,
  input  DB2,
  input  DB3,
  input  DB4,
  input  DB5,
  input  DB6,
  input  DB7,
  input  nW0,
  input  nW5_2,
  input  nW6_1,
  input  nW5_1,
  input  nW6_2,
  input  nDBE,
  input  RC,
  output THO0,
  output THO1,
  output THO2,
  output THO3,
  output THO4,
  output TVO1,
  output PA0,
  output PA1,
  output PA2,
  output PA3,
  output PA4,
  output PA5,
  output PA6,
  output PA7,
  output PA8,
  output PA9,
  output PA10,
  output PA11,
  output PA12,
  output FH0,
  output PA13,
  output FH1,
  output FH2
);

  wire _3_2_out, _3_out, _4_out, _6_2_out, _6_out, _10_out, _11_out, _14_out, _15_out, and_1_out, and_2_out,
       controlled_buffer_1_out, controlled_buffer_2_out, controlled_buffer_3_out, controlled_buffer_4_out,
       controlled_buffer_5_out, controlled_buffer_6_out, controlled_buffer_8_out, controlled_buffer_10_out,
       controlled_buffer_12_out, controlled_buffer_14_out, controlled_buffer_16_out,
       controlled_buffer_18_out, controlled_buffer_20_out, controlled_buffer_22_out,
       controlled_buffer_24_out, controlled_buffer_28_out, controlled_buffer_30_out,
       controlled_buffer_32_out, d_latch_1_q, d_latch_2_not_q, d_latch_3_not_q, d_latch_4_not_q, d_latch_5_q,
       d_latch_6_q, d_latch_7_q, DBE, multiplexer_1_out, multiplexer_2_out, multiplexer_3_out,
       multiplexer_4_out, multiplexer_5_out, multiplexer_6_out, multiplexer_7_out, multiplexer_8_out,
       multiplexer_9_out, multiplexer_10_out, multiplexer_11_out, multiplexer_12_out, multiplexer_13_out,
       multiplexer_14_out, multiplexer_15_out, multiplexer_16_out, multiplexer_17_out, multiplexer_18_out,
       multiplexer_19_out, multiplexer_20_out, multiplexer_21_out, multiplexer_22_out, multiplexer_23_out,
       multiplexer_24_out, multiplexer_25_out, multiplexer_26_out, multiplexer_27_out, multiplexer_28_out,
       multiplexer_29_out, multiplexer_30_out, multiplexer_31_out, multiplexer_32_out, multiplexer_33_out,
       multiplexer_34_out, multiplexer_35_out, multiplexer_36_out, multiplexer_37_out, multiplexer_38_out,
       multiplexer_39_out, multiplexer_40_out, multiplexer_41_out, multiplexer_42_out, multiplexer_43_out,
       multiplexer_44_out, multiplexer_45_out, n3bit_counter_1_q0, n3bit_counter_1_q1, n3bit_counter_1_q2,
       n3bit_counter_1_txz, n5_bit_counter_1_txz, n5_bit_counter_1_txzb, n5_bit_counter_2_q0,
       n5_bit_counter_2_q2, n5_bit_counter_2_q3, n5_bit_counter_2_q4, n5_bit_counter_2_txz,
       n5_bit_counter_2_txzb, nand_1_out, nor_1_out, nor_2_out, nor_8_out, nor_9_out, nor_10_out, nor_14_out,
       nor_15_out, nor_16_out, nor_17_out, nor_18_out, nor_19_out, nor_20_out, nor_21_out, nor_22_out,
       nor_23_out, nor_24_out, nor_25_out, nor_26_out, nor_27_out, nor_28_out, nor_29_out, nor_30_out,
       nor_31_out, not_3_out, not_4_out, not_5_out, not_6_out, not_7_out, not_8_out, nPCLK, nW0_prime,
       nW5_1_prime, nW5_2_prime, nW6_1_prime, nW6_2_prime, or_1_out, or_2_out, or_3_out,
       par_1bit_counter_1_carry_out, par_1bit_counter_1_q, par_1bit_counter_2_carry_out,
       par_1bit_counter_2_q, pattern_readout_1_pad0, pattern_readout_1_pad1, pattern_readout_1_pad2,
       pattern_readout_1_pad3, pattern_readout_1_pad4, pattern_readout_1_pad5, pattern_readout_1_pad6,
       pattern_readout_1_pad7, pattern_readout_1_pad8, pattern_readout_1_pad9, pattern_readout_1_pad10,
       pattern_readout_1_pad11, pattern_readout_1_pad12, pattern_readout_1_parr;
  wire [2:0] n3bit_counter_1_nq0;

  not not_1 (nPCLK, PCLK);
  D_latch d_latch_1 (.EN(PCLK), .D(SC_CNT), .Q(d_latch_1_q));  // open: NOT_Q
  D_latch d_latch_2 (.EN(nPCLK), .D(E_EV), .NOT_Q(d_latch_2_not_q));  // open: Q
  nor nor_1 (nor_1_out, E_EV, TSTEP);
  nor nor_2 (nor_2_out, TSTEP, and_1_out);
  and and_1 (and_1_out, F_TB, H0_prime_prime);
  nor nor_3 (nW0_prime, nW0, nDBE);
  nor nor_4 (nW5_2_prime, nW5_2, nDBE);
  nor nor_5 (nW6_1_prime, nW6_1, nDBE);
  nor nor_6 (nW5_1_prime, nW5_1, nDBE);
  nor nor_7 (nW6_2_prime, nW6_2, nDBE);
  not not_2 (DBE, nDBE);
  and _3 (_3_out, d_latch_1_q, RESCL);
  D_latch d_latch_3 (.EN(PCLK), .D(d_latch_2_not_q), .NOT_Q(d_latch_3_not_q));  // open: Q
  nor nor_8 (nor_8_out, nor_1_out, PCLK);
  nor nor_9 (nor_9_out, PCLK, nor_2_out);
  D_latch d_latch_4 (.EN(PCLK), .D(n5_bit_counter_2_txzb), .NOT_Q(d_latch_4_not_q));  // open: Q
  assign controlled_buffer_1_out = nW5_1_prime ? DB0 : 1'bz;  // Controlled_Buffer controlled_buffer_1
  assign controlled_buffer_2_out = nW5_1_prime ? DB1 : 1'bz;  // Controlled_Buffer controlled_buffer_2
  assign controlled_buffer_3_out = nW5_1_prime ? DB2 : 1'bz;  // Controlled_Buffer controlled_buffer_3
  D_latch d_latch_5 (.EN(PCLK), .D(not_3_out), .Q(d_latch_5_q));  // open: NOT_Q
  D_latch d_latch_6 (.EN(nPCLK), .D(d_latch_4_not_q), .Q(d_latch_6_q));  // open: NOT_Q
  Multiplexer #(.disabled(0), .enable("false")) multiplexer_1 (
    .in0(FH0), .in1(controlled_buffer_1_out), .out(multiplexer_1_out), .sel(DBE));
  Multiplexer #(.disabled(0), .enable("false")) multiplexer_2 (
    .in0(FH1), .in1(controlled_buffer_2_out), .out(multiplexer_2_out), .sel(DBE));
  Multiplexer #(.disabled(0), .enable("false")) multiplexer_3 (
    .in0(FH2), .in1(controlled_buffer_3_out), .out(multiplexer_3_out), .sel(DBE));
  and _6 (_6_out, nPCLK, d_latch_7_q);
  not not_3 (not_3_out, nor_8_out);
  nor nor_10 (nor_10_out, d_latch_5_q, d_latch_6_q);
  nor nor_11 (FH0, RC, ~multiplexer_1_out);  // NOR_Gate
  Pull_Resistor pull_resistor_1 (.node(multiplexer_1_out));
  nor nor_12 (FH1, RC, ~multiplexer_2_out);  // NOR_Gate
  Pull_Resistor pull_resistor_2 (.node(multiplexer_2_out));
  nor nor_13 (FH2, RC, ~multiplexer_3_out);  // NOR_Gate
  Pull_Resistor pull_resistor_3 (.node(multiplexer_3_out));
  nor _6_2 (_6_2_out, _6_out, _10_out);
  nor _10 (_10_out, _6_2_out, nW6_2_prime);
  nor _11 (_11_out, _10_out, nW6_2_prime);
  and and_2 (and_2_out, l1_32, BLNK);
  Multiplexer #(.disabled(0), .enable("false")) multiplexer_4 (
    .in0(_11_out), .in1(not_4_out), .out(multiplexer_4_out), .sel(PCLK));
  not not_4 (not_4_out, not_5_out);
  nand nand_1 (nand_1_out, BLNK, l1_32);
  not not_5 (not_5_out, multiplexer_4_out);
  or or_1 (or_1_out, n5_bit_counter_1_txz, and_2_out, n3bit_counter_1_txz);
  assign controlled_buffer_4_out = nW0_prime ? DB0 : 1'bz;  // Controlled_Buffer controlled_buffer_4
  assign controlled_buffer_5_out = nW0_prime ? DB1 : 1'bz;  // Controlled_Buffer controlled_buffer_5
  D_latch d_latch_7 (.EN(PCLK), .D(not_4_out), .Q(d_latch_7_q));  // open: NOT_Q
  assign controlled_buffer_6_out = nW6_2_prime ? DB0 : 1'bz;  // Controlled_Buffer controlled_buffer_6
  assign controlled_buffer_6_out = nW5_1_prime ? DB3 : 1'bz;  // Controlled_Buffer controlled_buffer_7
  assign controlled_buffer_8_out = nW6_2_prime ? DB1 : 1'bz;  // Controlled_Buffer controlled_buffer_8
  assign controlled_buffer_8_out = nW5_1_prime ? DB4 : 1'bz;  // Controlled_Buffer controlled_buffer_9
  assign controlled_buffer_10_out = nW6_2_prime ? DB2 : 1'bz;  // Controlled_Buffer controlled_buffer_10
  assign controlled_buffer_10_out = nW5_1_prime ? DB5 : 1'bz;  // Controlled_Buffer controlled_buffer_11
  assign controlled_buffer_12_out = nW6_2_prime ? DB3 : 1'bz;  // Controlled_Buffer controlled_buffer_12
  assign controlled_buffer_12_out = nW5_1_prime ? DB6 : 1'bz;  // Controlled_Buffer controlled_buffer_13
  assign controlled_buffer_14_out = nW6_2_prime ? DB4 : 1'bz;  // Controlled_Buffer controlled_buffer_14
  assign controlled_buffer_14_out = nW5_1_prime ? DB7 : 1'bz;  // Controlled_Buffer controlled_buffer_15
  assign controlled_buffer_16_out = nW6_2_prime ? DB5 : 1'bz;  // Controlled_Buffer controlled_buffer_16
  assign controlled_buffer_16_out = nW5_2_prime ? DB3 : 1'bz;  // Controlled_Buffer controlled_buffer_17
  assign controlled_buffer_18_out = nW6_2_prime ? DB6 : 1'bz;  // Controlled_Buffer controlled_buffer_18
  assign controlled_buffer_18_out = nW5_2_prime ? DB4 : 1'bz;  // Controlled_Buffer controlled_buffer_19
  assign controlled_buffer_20_out = nW6_2_prime ? DB7 : 1'bz;  // Controlled_Buffer controlled_buffer_20
  assign controlled_buffer_20_out = nW5_2_prime ? DB5 : 1'bz;  // Controlled_Buffer controlled_buffer_21
  assign controlled_buffer_22_out = nW6_1_prime ? DB0 : 1'bz;  // Controlled_Buffer controlled_buffer_22
  assign controlled_buffer_22_out = nW5_2_prime ? DB6 : 1'bz;  // Controlled_Buffer controlled_buffer_23
  assign controlled_buffer_24_out = nW6_1_prime ? DB1 : 1'bz;  // Controlled_Buffer controlled_buffer_24
  assign controlled_buffer_24_out = nW5_2_prime ? DB7 : 1'bz;  // Controlled_Buffer controlled_buffer_25
  assign controlled_buffer_4_out = nW6_1_prime ? DB2 : 1'bz;  // Controlled_Buffer controlled_buffer_26
  assign controlled_buffer_5_out = nW6_1_prime ? DB3 : 1'bz;  // Controlled_Buffer controlled_buffer_27
  assign controlled_buffer_28_out = nW6_1_prime ? DB4 : 1'bz;  // Controlled_Buffer controlled_buffer_28
  assign controlled_buffer_28_out = nW5_2_prime ? DB0 : 1'bz;  // Controlled_Buffer controlled_buffer_29
  assign controlled_buffer_30_out = nW6_1_prime ? DB5 : 1'bz;  // Controlled_Buffer controlled_buffer_30
  assign controlled_buffer_30_out = nW5_2_prime ? DB1 : 1'bz;  // Controlled_Buffer controlled_buffer_31
  assign controlled_buffer_32_out = nW6_1_prime ? 1'b0 : 1'bz;  // Controlled_Buffer controlled_buffer_32
  assign controlled_buffer_32_out = nW5_2_prime ? DB2 : 1'bz;  // Controlled_Buffer controlled_buffer_33
  Multiplexer #(.disabled(0), .enable("false")) multiplexer_5 (
    .in0(nor_14_out), .in1(controlled_buffer_6_out), .out(multiplexer_5_out), .sel(DBE));
  Multiplexer #(.disabled(0), .enable("false")) multiplexer_6 (
    .in0(nor_15_out), .in1(controlled_buffer_8_out), .out(multiplexer_6_out), .sel(DBE));
  Multiplexer #(.disabled(0), .enable("false")) multiplexer_7 (
    .in0(nor_16_out), .in1(controlled_buffer_10_out), .out(multiplexer_7_out), .sel(DBE));
  Multiplexer #(.disabled(0), .enable("false")) multiplexer_8 (
    .in0(nor_17_out), .in1(controlled_buffer_12_out), .out(multiplexer_8_out), .sel(DBE));
  Multiplexer #(.enable("false")) multiplexer_9 (
    .in0(nor_18_out), .in1(controlled_buffer_14_out), .out(multiplexer_9_out), .sel(DBE));
  Multiplexer #(.enable("false")) multiplexer_10 (
    .in0(nor_19_out), .in1(controlled_buffer_16_out), .out(multiplexer_10_out), .sel(DBE));
  Multiplexer #(.enable("false")) multiplexer_11 (
    .in0(nor_20_out), .in1(controlled_buffer_18_out), .out(multiplexer_11_out), .sel(DBE));
  Multiplexer #(.enable("false")) multiplexer_12 (
    .in0(nor_21_out), .in1(controlled_buffer_20_out), .out(multiplexer_12_out), .sel(DBE));
  Multiplexer #(.enable("false")) multiplexer_13 (
    .in0(nor_22_out), .in1(controlled_buffer_22_out), .out(multiplexer_13_out), .sel(DBE));
  Multiplexer #(.enable("false")) multiplexer_14 (
    .in0(nor_23_out), .in1(controlled_buffer_24_out), .out(multiplexer_14_out), .sel(DBE));
  Multiplexer #(.enable("false")) multiplexer_15 (
    .in0(nor_24_out), .in1(controlled_buffer_4_out), .out(multiplexer_15_out), .sel(DBE));
  Multiplexer #(.enable("false")) multiplexer_16 (
    .in0(nor_25_out), .in1(controlled_buffer_5_out), .out(multiplexer_16_out), .sel(DBE));
  Multiplexer #(.enable("false")) multiplexer_17 (
    .in0(nor_26_out), .in1(controlled_buffer_28_out), .out(multiplexer_17_out), .sel(DBE));
  Multiplexer #(.disabled(0), .enable("false")) multiplexer_18 (
    .in0(nor_27_out), .in1(controlled_buffer_30_out), .out(multiplexer_18_out), .sel(DBE));
  Multiplexer #(.disabled(0), .enable("false")) multiplexer_19 (
    .in0(nor_28_out), .in1(controlled_buffer_32_out), .out(multiplexer_19_out), .sel(DBE));
  nor _3_2 (_3_2_out, _3_out, d_latch_7_q);
  nor _14 (_14_out, d_latch_7_q, d_latch_3_not_q);
  nor nor_14 (nor_14_out, RC, ~multiplexer_5_out);  // NOR_Gate
  Pull_Resistor pull_resistor_4 (.node(multiplexer_5_out));
  nor nor_15 (nor_15_out, RC, ~multiplexer_6_out);  // NOR_Gate
  Pull_Resistor pull_resistor_5 (.node(multiplexer_6_out));
  nor nor_16 (nor_16_out, RC, ~multiplexer_7_out);  // NOR_Gate
  Pull_Resistor pull_resistor_6 (.node(multiplexer_7_out));
  nor nor_17 (nor_17_out, RC, ~multiplexer_8_out);  // NOR_Gate
  Pull_Resistor pull_resistor_7 (.node(multiplexer_8_out));
  nor nor_18 (nor_18_out, RC, ~multiplexer_9_out);  // NOR_Gate
  Pull_Resistor pull_resistor_8 (.node(multiplexer_9_out));
  nor nor_19 (nor_19_out, RC, ~multiplexer_10_out);  // NOR_Gate
  Pull_Resistor pull_resistor_9 (.node(multiplexer_10_out));
  nor nor_20 (nor_20_out, RC, ~multiplexer_11_out);  // NOR_Gate
  Pull_Resistor pull_resistor_10 (.node(multiplexer_11_out));
  nor nor_21 (nor_21_out, RC, ~multiplexer_12_out);  // NOR_Gate
  Pull_Resistor pull_resistor_11 (.node(multiplexer_12_out));
  nor nor_22 (nor_22_out, RC, ~multiplexer_13_out);  // NOR_Gate
  Pull_Resistor pull_resistor_12 (.node(multiplexer_13_out));
  nor nor_23 (nor_23_out, RC, ~multiplexer_14_out);  // NOR_Gate
  Pull_Resistor pull_resistor_13 (.node(multiplexer_14_out));
  nor nor_24 (nor_24_out, RC, ~multiplexer_15_out);  // NOR_Gate
  Pull_Resistor pull_resistor_14 (.node(multiplexer_15_out));
  nor nor_25 (nor_25_out, RC, ~multiplexer_16_out);  // NOR_Gate
  Pull_Resistor pull_resistor_15 (.node(multiplexer_16_out));
  nor nor_26 (nor_26_out, RC, ~multiplexer_17_out);  // NOR_Gate
  Pull_Resistor pull_resistor_16 (.node(multiplexer_17_out));
  nor nor_27 (nor_27_out, RC, ~multiplexer_18_out);  // NOR_Gate
  Pull_Resistor pull_resistor_17 (.node(multiplexer_18_out));
  nor nor_28 (nor_28_out, RC, ~multiplexer_19_out);  // NOR_Gate
  Pull_Resistor pull_resistor_18 (.node(multiplexer_19_out));
  nor _4 (_4_out, PCLK, _3_2_out);
  nor _15 (_15_out, PCLK, _14_out);
  _5_BIT_COUNTER u_5_bit_counter_1 (
    .STEP(nor_9_out), .LOAD(_15_out), .PCLK(PCLK), .IN0(nor_14_out), .Q0(THO0), .RES(1'b0),
    .CARRY_IN(nand_1_out), .IN1(nor_15_out), .Q1(THO1), .IN2(nor_16_out), .Q2(THO2), .IN3(nor_17_out),
    .Q3(THO3), .IN4(nor_18_out), .Q4(THO4), .BLNK(BLNK), .TxZB(n5_bit_counter_1_txzb),
    .TxZ(n5_bit_counter_1_txz), .IN_NOR7_1(1'b1));
  _5_BIT_COUNTER u_5_bit_counter_2 (
    .STEP(nor_8_out), .LOAD(_4_out), .PCLK(PCLK), .IN0(nor_19_out), .Q0(n5_bit_counter_2_q0),
    .RES(nor_10_out), .CARRY_IN(or_1_out), .IN1(nor_20_out), .Q1(TVO1), .IN2(nor_21_out),
    .Q2(n5_bit_counter_2_q2), .IN3(nor_22_out), .Q3(n5_bit_counter_2_q3), .IN4(nor_23_out),
    .Q4(n5_bit_counter_2_q4), .BLNK(BLNK), .TxZB(n5_bit_counter_2_txzb), .TxZ(n5_bit_counter_2_txz),
    .IN_NOR7_1(or_1_out));
  PAR_1BIT_COUNTER par_1bit_counter_1 (
    .PCLK(PCLK), .IN(nor_24_out), .CARRY_IN(or_3_out), .LOAD(_15_out), .STEP(nor_9_out),
    .Q(par_1bit_counter_1_q), .CARRY_OUT(par_1bit_counter_1_carry_out), .RES(1'b0));
  PAR_1BIT_COUNTER par_1bit_counter_2 (
    .PCLK(PCLK), .IN(nor_25_out), .CARRY_IN(or_2_out), .LOAD(_4_out), .STEP(nor_8_out),
    .Q(par_1bit_counter_2_q), .CARRY_OUT(par_1bit_counter_2_carry_out), .RES(1'b0));
  _3BIT_COUNTER u_3bit_counter_1 (
    .TxZ(n3bit_counter_1_txz), .BLNK(BLNK), .STEP(nor_8_out), .LOAD(_4_out), .PCLK(PCLK), .IN0(nor_26_out),
    .Q0(n3bit_counter_1_q0), .nQ0(n3bit_counter_1_nq0[0]), .RES(1'b0), .CARRY_IN(not_6_out),
    .IN1(nor_27_out), .Q1(n3bit_counter_1_q1), .nQ1(n3bit_counter_1_nq0[1]), .IN2(nor_28_out),
    .Q2(n3bit_counter_1_q2), .nQ2(n3bit_counter_1_nq0[2]), ._111(nor_29_out));
  or or_2 (or_2_out, n5_bit_counter_2_txzb, multiplexer_20_out);
  or or_3 (or_3_out, n5_bit_counter_2_txz, n5_bit_counter_1_txzb);
  Multiplexer #(.enable("false")) multiplexer_20 (
    .in0(par_1bit_counter_1_carry_out), .in1(1'b0), .out(multiplexer_20_out), .sel(not_7_out));
  Multiplexer #(.enable("false")) multiplexer_21 (
    .in0(par_1bit_counter_2_carry_out), .in1(1'b0), .out(multiplexer_21_out), .sel(not_7_out));
  not not_6 (not_6_out, nor_29_out);
  nor nor_29 (nor_29_out, multiplexer_21_out, not_7_out);
  nor nor_30 (nor_30_out, not_7_out, n3bit_counter_1_nq0[0]);
  nor nor_31 (nor_31_out, not_7_out, n3bit_counter_1_q1);
  not not_7 (not_7_out, BLNK);
  not not_8 (not_8_out, nor_31_out);
  Multiplexer #(.enable("false")) multiplexer_22 (.in0(THO0), .in1(THO2), .out(multiplexer_22_out), .sel(F_AT));
  Multiplexer #(.enable("false")) multiplexer_23 (.in0(THO1), .in1(THO3), .out(multiplexer_23_out), .sel(F_AT));
  Multiplexer #(.enable("false")) multiplexer_24 (.in0(THO2), .in1(THO4), .out(multiplexer_24_out), .sel(F_AT));
  Multiplexer #(.enable("false")) multiplexer_25 (
    .in0(THO3), .in1(n5_bit_counter_2_q2), .out(multiplexer_25_out), .sel(F_AT));
  Multiplexer #(.enable("false")) multiplexer_26 (
    .in0(THO4), .in1(n5_bit_counter_2_q3), .out(multiplexer_26_out), .sel(F_AT));
  Multiplexer #(.enable("false")) multiplexer_27 (
    .in0(n5_bit_counter_2_q0), .in1(n5_bit_counter_2_q4), .out(multiplexer_27_out), .sel(F_AT));
  Multiplexer #(.enable("false")) multiplexer_28 (.in0(TVO1), .in1(1'b1), .out(multiplexer_28_out), .sel(F_AT));
  Multiplexer #(.enable("false")) multiplexer_29 (
    .in0(n5_bit_counter_2_q2), .in1(1'b1), .out(multiplexer_29_out), .sel(F_AT));
  Multiplexer #(.enable("false")) multiplexer_30 (
    .in0(n5_bit_counter_2_q3), .in1(1'b1), .out(multiplexer_30_out), .sel(F_AT));
  Multiplexer #(.enable("false")) multiplexer_31 (
    .in0(n5_bit_counter_2_q4), .in1(1'b1), .out(multiplexer_31_out), .sel(F_AT));
  Multiplexer #(.enable("false")) multiplexer_32 (
    .in0(multiplexer_22_out), .in1(pattern_readout_1_pad0), .out(multiplexer_32_out),
    .sel(pattern_readout_1_parr));
  Multiplexer #(.enable("false")) multiplexer_33 (
    .in0(multiplexer_23_out), .in1(pattern_readout_1_pad1), .out(multiplexer_33_out),
    .sel(pattern_readout_1_parr));
  Multiplexer #(.enable("false")) multiplexer_34 (
    .in0(multiplexer_24_out), .in1(pattern_readout_1_pad2), .out(multiplexer_34_out),
    .sel(pattern_readout_1_parr));
  Multiplexer #(.enable("false")) multiplexer_35 (
    .in0(multiplexer_25_out), .in1(pattern_readout_1_pad3), .out(multiplexer_35_out),
    .sel(pattern_readout_1_parr));
  Multiplexer #(.enable("false")) multiplexer_36 (
    .in0(multiplexer_26_out), .in1(pattern_readout_1_pad4), .out(multiplexer_36_out),
    .sel(pattern_readout_1_parr));
  Multiplexer #(.enable("false")) multiplexer_37 (
    .in0(multiplexer_27_out), .in1(pattern_readout_1_pad5), .out(multiplexer_37_out),
    .sel(pattern_readout_1_parr));
  Multiplexer #(.enable("false")) multiplexer_38 (
    .in0(multiplexer_28_out), .in1(pattern_readout_1_pad6), .out(multiplexer_38_out),
    .sel(pattern_readout_1_parr));
  Multiplexer #(.enable("false")) multiplexer_39 (
    .in0(multiplexer_29_out), .in1(pattern_readout_1_pad7), .out(multiplexer_39_out),
    .sel(pattern_readout_1_parr));
  Multiplexer #(.enable("false")) multiplexer_40 (
    .in0(multiplexer_30_out), .in1(pattern_readout_1_pad8), .out(multiplexer_40_out),
    .sel(pattern_readout_1_parr));
  Multiplexer #(.enable("false")) multiplexer_41 (
    .in0(multiplexer_31_out), .in1(pattern_readout_1_pad9), .out(multiplexer_41_out),
    .sel(pattern_readout_1_parr));
  Multiplexer #(.enable("false")) multiplexer_42 (
    .in0(par_1bit_counter_1_q), .in1(pattern_readout_1_pad10), .out(multiplexer_42_out),
    .sel(pattern_readout_1_parr));
  Multiplexer #(.enable("false")) multiplexer_43 (
    .in0(par_1bit_counter_2_q), .in1(pattern_readout_1_pad11), .out(multiplexer_43_out),
    .sel(pattern_readout_1_parr));
  Multiplexer #(.enable("false")) multiplexer_44 (
    .in0(nor_30_out), .in1(pattern_readout_1_pad12), .out(multiplexer_44_out), .sel(pattern_readout_1_parr));
  Multiplexer #(.enable("false")) multiplexer_45 (
    .in0(not_8_out), .in1(1'b0), .out(multiplexer_45_out), .sel(pattern_readout_1_parr));
  D_latch d_latch_8 (.EN(PCLK), .D(multiplexer_32_out), .Q(PA0));  // open: NOT_Q
  D_latch d_latch_9 (.EN(PCLK), .D(multiplexer_33_out), .Q(PA1));  // open: NOT_Q
  D_latch d_latch_10 (.EN(PCLK), .D(multiplexer_34_out), .Q(PA2));  // open: NOT_Q
  D_latch d_latch_11 (.EN(PCLK), .D(multiplexer_35_out), .Q(PA3));  // open: NOT_Q
  D_latch d_latch_12 (.EN(PCLK), .D(multiplexer_36_out), .Q(PA4));  // open: NOT_Q
  D_latch d_latch_13 (.EN(PCLK), .D(multiplexer_37_out), .Q(PA5));  // open: NOT_Q
  D_latch d_latch_14 (.EN(PCLK), .D(multiplexer_38_out), .Q(PA6));  // open: NOT_Q
  D_latch d_latch_15 (.EN(PCLK), .D(multiplexer_39_out), .Q(PA7));  // open: NOT_Q
  D_latch d_latch_16 (.EN(PCLK), .D(multiplexer_40_out), .Q(PA8));  // open: NOT_Q
  D_latch d_latch_17 (.EN(PCLK), .D(multiplexer_41_out), .Q(PA9));  // open: NOT_Q
  D_latch d_latch_18 (.EN(PCLK), .D(multiplexer_42_out), .Q(PA10));  // open: NOT_Q
  D_latch d_latch_19 (.EN(PCLK), .D(multiplexer_43_out), .Q(PA11));  // open: NOT_Q
  D_latch d_latch_20 (.EN(PCLK), .D(multiplexer_44_out), .Q(PA12));  // open: NOT_Q
  D_latch d_latch_21 (.EN(PCLK), .D(multiplexer_45_out), .Q(PA13));  // open: NOT_Q
  PATTERN_READOUT pattern_readout_1 (
    .PD7(PD7), .OB7(OB7), .PD6(PD6), .OB6(OB6), .PD5(PD5), .OB5(OB5), .PD4(PD4), .OB4(OB4), .PD3(PD3),
    .OB3(OB3), .PD2(PD2), .OB2(OB2), .PD1(PD1), .OB1(OB1), .PD0(PD0), .OB0(OB0), .PCLK(PCLK), .OV3(OV3),
    .OV2(OV2), .OV1(OV1), .OV0(OV0), .OBSEL(OBSEL), .BGBSEL(BGSEL), .PAR_O(PAR_O), .O8_16(O8_16),
    .FVO2(n3bit_counter_1_nq0[2]), .FVO1(n3bit_counter_1_nq0[1]), .FVO0(n3bit_counter_1_nq0[0]), .SH2(SH2),
    .F_NT(F_NT), .H0_prime_prime(H0_prime_prime), .H2_prime(H2_prime), .PAD12(pattern_readout_1_pad12),
    .PAD0(pattern_readout_1_pad0), .PAD1(pattern_readout_1_pad1), .PAD2(pattern_readout_1_pad2),
    .PAD4(pattern_readout_1_pad4), .PAD5(pattern_readout_1_pad5), .PAD6(pattern_readout_1_pad6),
    .PAD7(pattern_readout_1_pad7), .PAD8(pattern_readout_1_pad8), .PAD9(pattern_readout_1_pad9),
    .PAD10(pattern_readout_1_pad10), .PAD11(pattern_readout_1_pad11), .PAD3(pattern_readout_1_pad3),
    .H1_prime(H1_prime), .BLNK(BLNK), .PARR(pattern_readout_1_parr));

  // Other names for the same wires on the sheet: OBJ_DATA[7:0] = {OB7, OB6, OB5, OB4, OB3, OB2, OB1, OB0};
  //   OV_DATA[3:0] = {OV3, OV2, OV1, OV0}; PPU_DATA[7:0] = {PD7, PD6, PD5, PD4, PD3, PD2, PD1, PD0}

  // Notes on the sheet:
  //   2
  //   13
  //   12
  //   TVZB
  //   E/EV''
  //   TVSTEP
  //   THSTEP
  //   TVZB''
  //   TVSTEP
  //   0/TV
  //   THIN
  //   OR
  //   8
  //   /W5/1'
  //   TVIN
  //   /W5/2'
  //   /W6/2'
  //   /W6/1'
  //   TVLOAD
  //   THLOAD
  //   TVIN
  //   NTH
  //   THSTEP
  //   THLOAD
  //   NTV
  //   TVSTEP
  //   TVLOAD
  //   TVSTEP
  //   TVLOAD
  //   THIN
  //   THLOAD
  //   THSTEP
  //   TH0
  //   TH1
  //   TH2
  //   TH3
  //   TH4
  //   TVLOAD
  //   TVSTEP
  //   TV0
  //   TV1
  //   TV2
  //   TV3
  //   TV4
  //   0/TV
  //   FV0
  //   FV1
  //   FV2
  //   THZ
  //   TVZB
  //   OR
  //   NTHIN
  //   TVZB
  //   TVZ
  //   NTH0
  //   NTVIN
  //   NTV0
  //   FVIN
  //   FVO0
  //   FVO1
  //   FVO2
  //   THZB
  //   /BLNK
  //   /BLNK
  //   /BLNK
  //   NTV0
  //   F/AT
  //   F/AT
  //   PARR
endmodule

module OAM_FIFO (
  input  PCLK,
  input  _0_HPOS,
  input  H3_prime_prime,
  input  H4_prime_prime,
  input  H5_prime_prime,
  input  SH2,
  input  SH3,
  input  SH5,
  input  SH7,
  input  nVIS,
  input  CLPO,
  input  OB0,
  input  OB1,
  input  OB2,
  input  OB3,
  input  OB4,
  input  OB5,
  input  OB6,
  input  OB7,
  input  T0,
  input  T1,
  input  T2,
  input  T3,
  input  T4,
  input  T5,
  input  T6,
  input  T7,
  output SPR0HIT,
  output ZCOL0,
  output ZCOL1,
  output ZCOL2,
  output ZCOL3,
  output ZPRIO
);

  wire _0_H, d_latch_1_not_q, d_latch_2_not_q, fifo_pipeline_1_x_col0, fifo_pipeline_1_x_col1,
       fifo_pipeline_1_x_col2, fifo_pipeline_1_x_col3, fifo_pipeline_1_x_en, fifo_pipeline_1_x_prio,
       fifo_pipeline_2_x_col0, fifo_pipeline_2_x_col1, fifo_pipeline_2_x_col2, fifo_pipeline_2_x_col3,
       fifo_pipeline_2_x_en, fifo_pipeline_2_x_prio, fifo_pipeline_3_x_col0, fifo_pipeline_3_x_col1,
       fifo_pipeline_3_x_col2, fifo_pipeline_3_x_col3, fifo_pipeline_3_x_en, fifo_pipeline_3_x_prio,
       fifo_pipeline_4_x_col0, fifo_pipeline_4_x_col1, fifo_pipeline_4_x_col2, fifo_pipeline_4_x_col3,
       fifo_pipeline_4_x_en, fifo_pipeline_4_x_prio, fifo_pipeline_5_x_col0, fifo_pipeline_5_x_col1,
       fifo_pipeline_5_x_col2, fifo_pipeline_5_x_col3, fifo_pipeline_5_x_en, fifo_pipeline_5_x_prio,
       fifo_pipeline_6_x_col0, fifo_pipeline_6_x_col1, fifo_pipeline_6_x_col2, fifo_pipeline_6_x_col3,
       fifo_pipeline_6_x_en, fifo_pipeline_6_x_prio, fifo_pipeline_7_x_col0, fifo_pipeline_7_x_col1,
       fifo_pipeline_7_x_col2, fifo_pipeline_7_x_col3, fifo_pipeline_7_x_en, fifo_pipeline_7_x_prio,
       fifo_pipeline_8_x_col0, fifo_pipeline_8_x_col1, fifo_pipeline_8_x_col2, fifo_pipeline_8_x_col3,
       fifo_pipeline_8_x_en, fifo_pipeline_8_x_prio, nH3_prime_prime, nH4_prime_prime, nH5_prime_prime,
       nor_1_out, nor_2_out, nor_3_out, nor_4_out, nor_5_out, nor_6_out, nor_7_out, nor_8_out, nor_9_out,
       nor_10_out, nor_11_out, nor_12_out, nor_13_out, nor_14_out, nor_15_out, nor_16_out, not_1_out;

  not not_1 (not_1_out, PCLK);
  not not_2 (nH3_prime_prime, H3_prime_prime);
  not not_3 (nH4_prime_prime, H4_prime_prime);
  not not_4 (nH5_prime_prime, H5_prime_prime);
  D_latch d_latch_1 (.EN(not_1_out), .D(_0_HPOS), .NOT_Q(d_latch_1_not_q));  // open: Q
  D_latch d_latch_2 (.EN(PCLK), .D(d_latch_1_not_q), .NOT_Q(d_latch_2_not_q));  // open: Q
  D_latch d_latch_3 (.EN(not_1_out), .D(d_latch_2_not_q), .NOT_Q(_0_H));  // open: Q
  FIFO_PIPELINE fifo_pipeline_1 (
    .PCLK(PCLK), .X_EN(fifo_pipeline_1_x_en), .SEL(nor_1_out), .SH5(SH5), .SH7(SH7), .SH3(SH3), ._0_H(_0_H),
    .nVIS(nVIS), .OB0(OB0), .OB1(OB1), .OB2(OB2), .OB3(OB3), .OB4(OB4), .OB5(OB5), .OB6(OB6), .OB7(OB7),
    .SH2(SH2), .X_COL0(fifo_pipeline_1_x_col0), .X_COL1(fifo_pipeline_1_x_col1),
    .X_COL2(fifo_pipeline_1_x_col2), .X_COL3(fifo_pipeline_1_x_col3), .X_PRIO(fifo_pipeline_1_x_prio),
    .T0(T0), .T1(T1), .T2(T2), .T3(T3), .T4(T4), .T5(T5), .T6(T6), .T7(T7));
  nor nor_1 (nor_1_out, H3_prime_prime, H4_prime_prime, H5_prime_prime);
  FIFO_PIPELINE fifo_pipeline_2 (
    .PCLK(PCLK), .X_EN(fifo_pipeline_2_x_en), .SEL(nor_2_out), .SH5(SH5), .SH7(SH7), .SH3(SH3), ._0_H(_0_H),
    .nVIS(nVIS), .OB0(OB0), .OB1(OB1), .OB2(OB2), .OB3(OB3), .OB4(OB4), .OB5(OB5), .OB6(OB6), .OB7(OB7),
    .SH2(SH2), .X_COL0(fifo_pipeline_2_x_col0), .X_COL1(fifo_pipeline_2_x_col1),
    .X_COL2(fifo_pipeline_2_x_col2), .X_COL3(fifo_pipeline_2_x_col3), .X_PRIO(fifo_pipeline_2_x_prio),
    .T0(T0), .T1(T1), .T2(T2), .T3(T3), .T4(T4), .T5(T5), .T6(T6), .T7(T7));
  nor nor_2 (nor_2_out, nH3_prime_prime, H4_prime_prime, H5_prime_prime);
  FIFO_PIPELINE fifo_pipeline_3 (
    .PCLK(PCLK), .X_EN(fifo_pipeline_3_x_en), .SEL(nor_3_out), .SH5(SH5), .SH7(SH7), .SH3(SH3), ._0_H(_0_H),
    .nVIS(nVIS), .OB0(OB0), .OB1(OB1), .OB2(OB2), .OB3(OB3), .OB4(OB4), .OB5(OB5), .OB6(OB6), .OB7(OB7),
    .SH2(SH2), .X_COL0(fifo_pipeline_3_x_col0), .X_COL1(fifo_pipeline_3_x_col1),
    .X_COL2(fifo_pipeline_3_x_col2), .X_COL3(fifo_pipeline_3_x_col3), .X_PRIO(fifo_pipeline_3_x_prio),
    .T0(T0), .T1(T1), .T2(T2), .T3(T3), .T4(T4), .T5(T5), .T6(T6), .T7(T7));
  nor nor_3 (nor_3_out, H3_prime_prime, nH4_prime_prime, H5_prime_prime);
  FIFO_PIPELINE fifo_pipeline_4 (
    .PCLK(PCLK), .X_EN(fifo_pipeline_4_x_en), .SEL(nor_4_out), .SH5(SH5), .SH7(SH7), .SH3(SH3), ._0_H(_0_H),
    .nVIS(nVIS), .OB0(OB0), .OB1(OB1), .OB2(OB2), .OB3(OB3), .OB4(OB4), .OB5(OB5), .OB6(OB6), .OB7(OB7),
    .SH2(SH2), .X_COL0(fifo_pipeline_4_x_col0), .X_COL1(fifo_pipeline_4_x_col1),
    .X_COL2(fifo_pipeline_4_x_col2), .X_COL3(fifo_pipeline_4_x_col3), .X_PRIO(fifo_pipeline_4_x_prio),
    .T0(T0), .T1(T1), .T2(T2), .T3(T3), .T4(T4), .T5(T5), .T6(T6), .T7(T7));
  nor nor_4 (nor_4_out, nH3_prime_prime, nH4_prime_prime, H5_prime_prime);
  FIFO_PIPELINE fifo_pipeline_5 (
    .PCLK(PCLK), .X_EN(fifo_pipeline_5_x_en), .SEL(nor_5_out), .SH5(SH5), .SH7(SH7), .SH3(SH3), ._0_H(_0_H),
    .nVIS(nVIS), .OB0(OB0), .OB1(OB1), .OB2(OB2), .OB3(OB3), .OB4(OB4), .OB5(OB5), .OB6(OB6), .OB7(OB7),
    .SH2(SH2), .X_COL0(fifo_pipeline_5_x_col0), .X_COL1(fifo_pipeline_5_x_col1),
    .X_COL2(fifo_pipeline_5_x_col2), .X_COL3(fifo_pipeline_5_x_col3), .X_PRIO(fifo_pipeline_5_x_prio),
    .T0(T0), .T1(T1), .T2(T2), .T3(T3), .T4(T4), .T5(T5), .T6(T6), .T7(T7));
  nor nor_5 (nor_5_out, H3_prime_prime, H4_prime_prime, nH5_prime_prime);
  FIFO_PIPELINE fifo_pipeline_6 (
    .PCLK(PCLK), .X_EN(fifo_pipeline_6_x_en), .SEL(nor_6_out), .SH5(SH5), .SH7(SH7), .SH3(SH3), ._0_H(_0_H),
    .nVIS(nVIS), .OB0(OB0), .OB1(OB1), .OB2(OB2), .OB3(OB3), .OB4(OB4), .OB5(OB5), .OB6(OB6), .OB7(OB7),
    .SH2(SH2), .X_COL0(fifo_pipeline_6_x_col0), .X_COL1(fifo_pipeline_6_x_col1),
    .X_COL2(fifo_pipeline_6_x_col2), .X_COL3(fifo_pipeline_6_x_col3), .X_PRIO(fifo_pipeline_6_x_prio),
    .T0(T0), .T1(T1), .T2(T2), .T3(T3), .T4(T4), .T5(T5), .T6(T6), .T7(T7));
  nor nor_6 (nor_6_out, nH3_prime_prime, H4_prime_prime, nH5_prime_prime);
  FIFO_PIPELINE fifo_pipeline_7 (
    .PCLK(PCLK), .X_EN(fifo_pipeline_7_x_en), .SEL(nor_7_out), .SH5(SH5), .SH7(SH7), .SH3(SH3), ._0_H(_0_H),
    .nVIS(nVIS), .OB0(OB0), .OB1(OB1), .OB2(OB2), .OB3(OB3), .OB4(OB4), .OB5(OB5), .OB6(OB6), .OB7(OB7),
    .SH2(SH2), .X_COL0(fifo_pipeline_7_x_col0), .X_COL1(fifo_pipeline_7_x_col1),
    .X_COL2(fifo_pipeline_7_x_col2), .X_COL3(fifo_pipeline_7_x_col3), .X_PRIO(fifo_pipeline_7_x_prio),
    .T0(T0), .T1(T1), .T2(T2), .T3(T3), .T4(T4), .T5(T5), .T6(T6), .T7(T7));
  nor nor_7 (nor_7_out, H3_prime_prime, nH4_prime_prime, nH5_prime_prime);
  FIFO_PIPELINE fifo_pipeline_8 (
    .PCLK(PCLK), .X_EN(fifo_pipeline_8_x_en), .SEL(nor_8_out), .SH5(SH5), .SH7(SH7), .SH3(SH3), ._0_H(_0_H),
    .nVIS(nVIS), .OB0(OB0), .OB1(OB1), .OB2(OB2), .OB3(OB3), .OB4(OB4), .OB5(OB5), .OB6(OB6), .OB7(OB7),
    .SH2(SH2), .X_COL0(fifo_pipeline_8_x_col0), .X_COL1(fifo_pipeline_8_x_col1),
    .X_COL2(fifo_pipeline_8_x_col2), .X_COL3(fifo_pipeline_8_x_col3), .X_PRIO(fifo_pipeline_8_x_prio),
    .T0(T0), .T1(T1), .T2(T2), .T3(T3), .T4(T4), .T5(T5), .T6(T6), .T7(T7));
  nor nor_8 (nor_8_out, nH3_prime_prime, nH4_prime_prime, nH5_prime_prime);
  nor nor_9 (nor_9_out, CLPO, fifo_pipeline_1_x_en, fifo_pipeline_1_x_col1, fifo_pipeline_1_x_col0);
  nor nor_10 (nor_10_out, nor_9_out, CLPO, fifo_pipeline_2_x_en, fifo_pipeline_2_x_col1, fifo_pipeline_2_x_col0);
  nor nor_11 (nor_11_out, nor_10_out, nor_9_out, CLPO, fifo_pipeline_3_x_en, fifo_pipeline_3_x_col1, fifo_pipeline_3_x_col0);
  nor nor_12 (nor_12_out, nor_11_out, nor_10_out, nor_9_out, CLPO, fifo_pipeline_4_x_en, fifo_pipeline_4_x_col1, fifo_pipeline_4_x_col0);
  assign ZCOL0 = nor_9_out ? fifo_pipeline_1_x_col0 : 1'bz;  // Controlled_Buffer controlled_buffer_1
  assign ZCOL1 = nor_9_out ? fifo_pipeline_1_x_col1 : 1'bz;  // Controlled_Buffer controlled_buffer_2
  assign ZCOL2 = nor_9_out ? fifo_pipeline_1_x_col2 : 1'bz;  // Controlled_Buffer controlled_buffer_3
  assign ZCOL3 = nor_9_out ? fifo_pipeline_1_x_col3 : 1'bz;  // Controlled_Buffer controlled_buffer_4
  assign ZPRIO = nor_9_out ? fifo_pipeline_1_x_prio : 1'bz;  // Controlled_Buffer controlled_buffer_5
  assign ZCOL0 = nor_10_out ? fifo_pipeline_2_x_col0 : 1'bz;  // Controlled_Buffer controlled_buffer_6
  assign ZCOL1 = nor_10_out ? fifo_pipeline_2_x_col1 : 1'bz;  // Controlled_Buffer controlled_buffer_7
  assign ZCOL2 = nor_10_out ? fifo_pipeline_2_x_col2 : 1'bz;  // Controlled_Buffer controlled_buffer_8
  assign ZCOL3 = nor_10_out ? fifo_pipeline_2_x_col3 : 1'bz;  // Controlled_Buffer controlled_buffer_9
  assign ZPRIO = nor_10_out ? fifo_pipeline_2_x_prio : 1'bz;  // Controlled_Buffer controlled_buffer_10
  assign ZCOL0 = nor_11_out ? fifo_pipeline_3_x_col0 : 1'bz;  // Controlled_Buffer controlled_buffer_11
  assign ZCOL1 = nor_11_out ? fifo_pipeline_3_x_col1 : 1'bz;  // Controlled_Buffer controlled_buffer_12
  assign ZCOL2 = nor_11_out ? fifo_pipeline_3_x_col2 : 1'bz;  // Controlled_Buffer controlled_buffer_13
  assign ZCOL3 = nor_11_out ? fifo_pipeline_3_x_col3 : 1'bz;  // Controlled_Buffer controlled_buffer_14
  assign ZPRIO = nor_11_out ? fifo_pipeline_3_x_prio : 1'bz;  // Controlled_Buffer controlled_buffer_15
  assign ZCOL0 = nor_12_out ? fifo_pipeline_4_x_col0 : 1'bz;  // Controlled_Buffer controlled_buffer_16
  assign ZCOL1 = nor_12_out ? fifo_pipeline_4_x_col1 : 1'bz;  // Controlled_Buffer controlled_buffer_17
  assign ZCOL2 = nor_12_out ? fifo_pipeline_4_x_col2 : 1'bz;  // Controlled_Buffer controlled_buffer_18
  assign ZCOL3 = nor_12_out ? fifo_pipeline_4_x_col3 : 1'bz;  // Controlled_Buffer controlled_buffer_19
  assign ZPRIO = nor_12_out ? fifo_pipeline_4_x_prio : 1'bz;  // Controlled_Buffer controlled_buffer_20
  nor nor_13 (nor_13_out, nor_12_out, nor_11_out, nor_10_out, nor_9_out, CLPO, fifo_pipeline_5_x_en, fifo_pipeline_5_x_col1, fifo_pipeline_5_x_col0);
  assign ZCOL0 = nor_13_out ? fifo_pipeline_5_x_col0 : 1'bz;  // Controlled_Buffer controlled_buffer_21
  assign ZCOL1 = nor_13_out ? fifo_pipeline_5_x_col1 : 1'bz;  // Controlled_Buffer controlled_buffer_22
  assign ZCOL2 = nor_13_out ? fifo_pipeline_5_x_col2 : 1'bz;  // Controlled_Buffer controlled_buffer_23
  assign ZCOL3 = nor_13_out ? fifo_pipeline_5_x_col3 : 1'bz;  // Controlled_Buffer controlled_buffer_24
  assign ZPRIO = nor_13_out ? fifo_pipeline_5_x_prio : 1'bz;  // Controlled_Buffer controlled_buffer_25
  nor nor_14 (nor_14_out, nor_13_out, nor_12_out, nor_11_out, nor_10_out, nor_9_out, CLPO, fifo_pipeline_6_x_en, fifo_pipeline_6_x_col1, fifo_pipeline_6_x_col0);
  assign ZCOL0 = nor_14_out ? fifo_pipeline_6_x_col0 : 1'bz;  // Controlled_Buffer controlled_buffer_26
  assign ZCOL1 = nor_14_out ? fifo_pipeline_6_x_col1 : 1'bz;  // Controlled_Buffer controlled_buffer_27
  assign ZCOL2 = nor_14_out ? fifo_pipeline_6_x_col2 : 1'bz;  // Controlled_Buffer controlled_buffer_28
  assign ZCOL3 = nor_14_out ? fifo_pipeline_6_x_col3 : 1'bz;  // Controlled_Buffer controlled_buffer_29
  assign ZPRIO = nor_14_out ? fifo_pipeline_6_x_prio : 1'bz;  // Controlled_Buffer controlled_buffer_30
  nor nor_15 (nor_15_out, nor_14_out, nor_13_out, nor_12_out, nor_11_out, nor_10_out, nor_9_out, CLPO, fifo_pipeline_7_x_en, fifo_pipeline_7_x_col1, fifo_pipeline_7_x_col0);
  assign ZCOL0 = nor_15_out ? fifo_pipeline_7_x_col0 : 1'bz;  // Controlled_Buffer controlled_buffer_31
  assign ZCOL1 = nor_15_out ? fifo_pipeline_7_x_col1 : 1'bz;  // Controlled_Buffer controlled_buffer_32
  assign ZCOL2 = nor_15_out ? fifo_pipeline_7_x_col2 : 1'bz;  // Controlled_Buffer controlled_buffer_33
  assign ZCOL3 = nor_15_out ? fifo_pipeline_7_x_col3 : 1'bz;  // Controlled_Buffer controlled_buffer_34
  assign ZPRIO = nor_15_out ? fifo_pipeline_7_x_prio : 1'bz;  // Controlled_Buffer controlled_buffer_35
  nor nor_16 (nor_16_out, nor_15_out, nor_14_out, nor_13_out, nor_12_out, nor_11_out, nor_10_out, nor_9_out, CLPO, fifo_pipeline_8_x_en, fifo_pipeline_8_x_col1, fifo_pipeline_8_x_col0);
  assign ZCOL0 = nor_16_out ? fifo_pipeline_8_x_col0 : 1'bz;  // Controlled_Buffer controlled_buffer_36
  assign ZCOL1 = nor_16_out ? fifo_pipeline_8_x_col1 : 1'bz;  // Controlled_Buffer controlled_buffer_37
  assign ZCOL2 = nor_16_out ? fifo_pipeline_8_x_col2 : 1'bz;  // Controlled_Buffer controlled_buffer_38
  assign ZCOL3 = nor_16_out ? fifo_pipeline_8_x_col3 : 1'bz;  // Controlled_Buffer controlled_buffer_39
  assign ZPRIO = nor_16_out ? fifo_pipeline_8_x_prio : 1'bz;  // Controlled_Buffer controlled_buffer_40
  D_latch d_latch_4 (.EN(PCLK), .D(nor_9_out), .NOT_Q(SPR0HIT));  // open: Q

  // Other names for the same wires on the sheet: OBJ_BUS[7:0] = {OB7, OB6, OB5, OB4, OB3, OB2, OB1, OB0};
  //   T_BUS[7:0] = {T7, T6, T5, T4, T3, T2, T1, T0}
endmodule

// PAR 1BIT COUNTER
module PAR_1BIT_COUNTER (
  input  STEP,
  input  LOAD,
  input  PCLK,
  input  IN,
  input  RES,
  input  CARRY_IN,
  output Q,
  output CARRY_OUT
);

  wire controlled_buffer_1_out, d_latch_1_not_q, d_latch_2_not_q, multiplexer_1_out, nor_1_out, not_1_out;

  nor nor_1 (nor_1_out, d_latch_2_not_q, RES);
  Multiplexer #(.enable("false")) multiplexer_1 (
    .in0(d_latch_2_not_q), .in1(nor_1_out), .out(multiplexer_1_out), .sel(CARRY_IN));
  D_latch d_latch_1 (.EN(PCLK), .D(multiplexer_1_out), .NOT_Q(d_latch_1_not_q));  // open: Q
  assign controlled_buffer_1_out = PCLK ? nor_1_out : 1'bz;  // Controlled_Buffer controlled_buffer_1
  not not_1 (not_1_out, CARRY_IN);
  assign controlled_buffer_1_out = LOAD ? IN : 1'bz;  // Controlled_Buffer controlled_buffer_2
  assign controlled_buffer_1_out = STEP ? d_latch_1_not_q : 1'bz;  // Controlled_Buffer controlled_buffer_3
  D_latch d_latch_2 (.EN(1'b1), .D(controlled_buffer_1_out), .Q(Q), .NOT_Q(d_latch_2_not_q));
  nor nor_2 (CARRY_OUT, d_latch_2_not_q, not_1_out);
endmodule

module READ__2007 (
  input  XRB,
  input  RC,
  input  PD_RB,
  input  PD0,
  input  PD1,
  input  PD2,
  input  PD3,
  input  PD4,
  input  PD5,
  input  PD6,
  input  PD7,
  output DB0,
  output DB1,
  output DB2,
  output DB3,
  output DB4,
  output DB5,
  output DB6,
  output DB7
);

  wire multiplexer_1_out, multiplexer_2_out, multiplexer_3_out, multiplexer_4_out, multiplexer_5_out,
       multiplexer_6_out, multiplexer_7_out, multiplexer_8_out, nor_1_out, nor_2_out, nor_3_out, nor_4_out,
       nor_5_out, nor_6_out, nor_7_out, nor_8_out, not_1_out, not_2_out, not_3_out, not_4_out, not_5_out,
       not_6_out, not_7_out, not_8_out, not_9_out;

  not not_1 (not_1_out, XRB);
  Multiplexer #(.enable("false")) multiplexer_1 (.in0(nor_1_out), .in1(PD0), .out(multiplexer_1_out), .sel(PD_RB));
  not not_2 (not_2_out, multiplexer_1_out);
  Multiplexer #(.enable("false")) multiplexer_2 (.in0(nor_2_out), .in1(PD1), .out(multiplexer_2_out), .sel(PD_RB));
  not not_3 (not_3_out, multiplexer_2_out);
  not not_4 (not_4_out, multiplexer_3_out);
  Multiplexer #(.enable("false")) multiplexer_3 (.in0(nor_3_out), .in1(PD2), .out(multiplexer_3_out), .sel(PD_RB));
  Multiplexer #(.enable("false")) multiplexer_4 (.in0(nor_4_out), .in1(PD3), .out(multiplexer_4_out), .sel(PD_RB));
  not not_5 (not_5_out, multiplexer_4_out);
  Multiplexer #(.enable("false")) multiplexer_5 (.in0(nor_5_out), .in1(PD4), .out(multiplexer_5_out), .sel(PD_RB));
  not not_6 (not_6_out, multiplexer_5_out);
  not not_7 (not_7_out, multiplexer_6_out);
  Multiplexer #(.enable("false")) multiplexer_6 (.in0(nor_6_out), .in1(PD5), .out(multiplexer_6_out), .sel(PD_RB));
  not not_8 (not_8_out, multiplexer_7_out);
  Multiplexer #(.enable("false")) multiplexer_7 (.in0(nor_7_out), .in1(PD6), .out(multiplexer_7_out), .sel(PD_RB));
  Multiplexer #(.enable("false")) multiplexer_8 (.in0(nor_8_out), .in1(PD7), .out(multiplexer_8_out), .sel(PD_RB));
  not not_9 (not_9_out, multiplexer_8_out);
  nor nor_1 (nor_1_out, not_2_out, RC);
  nor nor_2 (nor_2_out, not_3_out, RC);
  nor nor_3 (nor_3_out, not_4_out, RC);
  nor nor_4 (nor_4_out, not_5_out, RC);
  nor nor_5 (nor_5_out, not_6_out, RC);
  nor nor_6 (nor_6_out, not_7_out, RC);
  nor nor_7 (nor_7_out, not_8_out, RC);
  nor nor_8 (nor_8_out, not_9_out, RC);
  Multiplexer multiplexer_9 (.in0(1'b0), .in1(1'b1), .out(DB0), .sel(nor_1_out), .en(not_1_out));
  Multiplexer multiplexer_10 (.in0(1'b0), .in1(1'b1), .out(DB1), .sel(nor_2_out), .en(not_1_out));
  Multiplexer multiplexer_11 (.in0(1'b0), .in1(1'b1), .out(DB2), .sel(nor_3_out), .en(not_1_out));
  Multiplexer multiplexer_12 (.in0(1'b0), .in1(1'b1), .out(DB3), .sel(nor_4_out), .en(not_1_out));
  Multiplexer multiplexer_13 (.in0(1'b0), .in1(1'b1), .out(DB4), .sel(nor_5_out), .en(not_1_out));
  Multiplexer multiplexer_14 (.in0(1'b0), .in1(1'b1), .out(DB5), .sel(nor_6_out), .en(not_1_out));
  Multiplexer multiplexer_15 (.in0(1'b0), .in1(1'b1), .out(DB6), .sel(nor_7_out), .en(not_1_out));
  Multiplexer multiplexer_16 (.in0(1'b0), .in1(1'b1), .out(DB7), .sel(nor_8_out), .en(not_1_out));
endmodule

module _5_BIT_COUNTER (
  input  IN_NOR7_1,
  input  BLNK,
  input  STEP,
  input  LOAD,
  input  PCLK,
  input  IN0,
  input  RES,
  input  CARRY_IN,
  input  IN1,
  input  IN2,
  input  IN3,
  input  IN4,
  output TxZB,
  output TxZ,
  output Q0,
  output Q1,
  output Q2,
  output Q3,
  output Q4
);

  wire controlled_buffer_1_out, controlled_buffer_2_out, controlled_buffer_3_out, controlled_buffer_4_out,
       controlled_buffer_5_out, d_latch_1_not_q, d_latch_2_not_q, d_latch_3_not_q, d_latch_4_not_q,
       d_latch_5_not_q, d_latch_6_not_q, d_latch_7_not_q, d_latch_8_not_q, d_latch_9_not_q, d_latch_10_not_q,
       multiplexer_1_out, multiplexer_2_out, multiplexer_3_out, multiplexer_4_out, multiplexer_5_out,
       nor_1_out, nor_2_out, nor_3_out, nor_4_out, nor_5_out, nor_8_out, nor_9_out, nor_10_out, nor_11_out,
       not_1_out, not_2_out, not_3_out, not_4_out, not_5_out, not_6_out;

  nor nor_1 (nor_1_out, d_latch_6_not_q, RES);
  nor nor_2 (nor_2_out, d_latch_7_not_q, RES);
  nor nor_3 (nor_3_out, d_latch_8_not_q, RES);
  nor nor_4 (nor_4_out, d_latch_9_not_q, RES);
  nor nor_5 (nor_5_out, d_latch_10_not_q, RES);
  Multiplexer #(.enable("false")) multiplexer_1 (
    .in0(d_latch_6_not_q), .in1(nor_1_out), .out(multiplexer_1_out), .sel(CARRY_IN));
  Multiplexer #(.enable("false")) multiplexer_2 (
    .in0(d_latch_7_not_q), .in1(nor_2_out), .out(multiplexer_2_out), .sel(nor_8_out));
  Multiplexer #(.enable("false")) multiplexer_3 (
    .in0(d_latch_8_not_q), .in1(nor_3_out), .out(multiplexer_3_out), .sel(nor_9_out));
  Multiplexer #(.enable("false")) multiplexer_4 (
    .in0(d_latch_9_not_q), .in1(nor_4_out), .out(multiplexer_4_out), .sel(nor_10_out));
  Multiplexer #(.enable("false")) multiplexer_5 (
    .in0(d_latch_10_not_q), .in1(nor_5_out), .out(multiplexer_5_out), .sel(nor_11_out));
  assign controlled_buffer_1_out = PCLK ? nor_1_out : 1'bz;  // Controlled_Buffer controlled_buffer_1
  assign controlled_buffer_2_out = PCLK ? nor_2_out : 1'bz;  // Controlled_Buffer controlled_buffer_2
  assign controlled_buffer_3_out = PCLK ? nor_3_out : 1'bz;  // Controlled_Buffer controlled_buffer_3
  assign controlled_buffer_4_out = PCLK ? nor_4_out : 1'bz;  // Controlled_Buffer controlled_buffer_4
  assign controlled_buffer_5_out = PCLK ? nor_5_out : 1'bz;  // Controlled_Buffer controlled_buffer_5
  assign controlled_buffer_1_out = LOAD ? IN0 : 1'bz;  // Controlled_Buffer controlled_buffer_6
  D_latch d_latch_1 (.EN(PCLK), .D(multiplexer_1_out), .NOT_Q(d_latch_1_not_q));  // open: Q
  assign controlled_buffer_1_out = STEP ? d_latch_1_not_q : 1'bz;  // Controlled_Buffer controlled_buffer_7
  assign controlled_buffer_2_out = LOAD ? IN1 : 1'bz;  // Controlled_Buffer controlled_buffer_8
  D_latch d_latch_2 (.EN(PCLK), .D(multiplexer_2_out), .NOT_Q(d_latch_2_not_q));  // open: Q
  assign controlled_buffer_2_out = STEP ? d_latch_2_not_q : 1'bz;  // Controlled_Buffer controlled_buffer_9
  assign controlled_buffer_3_out = LOAD ? IN2 : 1'bz;  // Controlled_Buffer controlled_buffer_10
  D_latch d_latch_3 (.EN(PCLK), .D(multiplexer_3_out), .NOT_Q(d_latch_3_not_q));  // open: Q
  assign controlled_buffer_3_out = STEP ? d_latch_3_not_q : 1'bz;  // Controlled_Buffer controlled_buffer_11
  assign controlled_buffer_4_out = LOAD ? IN3 : 1'bz;  // Controlled_Buffer controlled_buffer_12
  D_latch d_latch_4 (.EN(PCLK), .D(multiplexer_4_out), .NOT_Q(d_latch_4_not_q));  // open: Q
  assign controlled_buffer_4_out = STEP ? d_latch_4_not_q : 1'bz;  // Controlled_Buffer controlled_buffer_13
  assign controlled_buffer_5_out = LOAD ? IN4 : 1'bz;  // Controlled_Buffer controlled_buffer_14
  D_latch d_latch_5 (.EN(PCLK), .D(multiplexer_5_out), .NOT_Q(d_latch_5_not_q));  // open: Q
  assign controlled_buffer_5_out = STEP ? d_latch_5_not_q : 1'bz;  // Controlled_Buffer controlled_buffer_15
  not not_1 (not_1_out, IN_NOR7_1);
  nor nor_6 (TxZ, d_latch_10_not_q, d_latch_9_not_q, d_latch_8_not_q, not_1_out, d_latch_7_not_q, d_latch_6_not_q, not_2_out);
  not not_2 (not_2_out, BLNK);
  nor nor_7 (TxZB, BLNK, d_latch_10_not_q, d_latch_9_not_q, not_1_out, d_latch_8_not_q, d_latch_7_not_q, d_latch_6_not_q);
  D_latch d_latch_6 (.EN(1'b1), .D(controlled_buffer_1_out), .Q(Q0), .NOT_Q(d_latch_6_not_q));
  nor nor_8 (nor_8_out, d_latch_6_not_q, not_3_out);
  not not_3 (not_3_out, CARRY_IN);
  D_latch d_latch_7 (.EN(1'b1), .D(controlled_buffer_2_out), .Q(Q1), .NOT_Q(d_latch_7_not_q));
  nor nor_9 (nor_9_out, d_latch_7_not_q, not_4_out);
  not not_4 (not_4_out, nor_8_out);
  D_latch d_latch_8 (.EN(1'b1), .D(controlled_buffer_3_out), .Q(Q2), .NOT_Q(d_latch_8_not_q));
  nor nor_10 (nor_10_out, d_latch_8_not_q, not_5_out);
  not not_5 (not_5_out, nor_9_out);
  D_latch d_latch_9 (.EN(1'b1), .D(controlled_buffer_4_out), .Q(Q3), .NOT_Q(d_latch_9_not_q));
  nor nor_11 (nor_11_out, d_latch_9_not_q, not_6_out);
  not not_6 (not_6_out, nor_10_out);
  D_latch d_latch_10 (.EN(1'b1), .D(controlled_buffer_5_out), .Q(Q4), .NOT_Q(d_latch_10_not_q));
endmodule

module _3BIT_COUNTER (
  input  _111,
  input  BLNK,
  input  STEP,
  input  LOAD,
  input  PCLK,
  input  IN0,
  input  RES,
  input  CARRY_IN,
  input  IN1,
  input  IN2,
  output TxZ,
  output Q0,
  output nQ0,
  output Q1,
  output nQ1,
  output Q2,
  output nQ2
);

  wire controlled_buffer_1_out, controlled_buffer_2_out, controlled_buffer_3_out, d_latch_1_not_q,
       d_latch_2_not_q, d_latch_3_not_q, multiplexer_1_out, multiplexer_2_out, multiplexer_3_out, nor_1_out,
       nor_2_out, nor_3_out, nor_5_out, nor_6_out, not_1_out, not_2_out;

  nor nor_1 (nor_1_out, nQ0, RES);
  nor nor_2 (nor_2_out, nQ1, RES);
  nor nor_3 (nor_3_out, nQ2, RES);
  Multiplexer #(.enable("false")) multiplexer_1 (.in0(nQ0), .in1(nor_1_out), .out(multiplexer_1_out), .sel(CARRY_IN));
  Multiplexer #(.enable("false")) multiplexer_2 (.in0(nQ1), .in1(nor_2_out), .out(multiplexer_2_out), .sel(nor_5_out));
  Multiplexer #(.enable("false")) multiplexer_3 (.in0(nQ2), .in1(nor_3_out), .out(multiplexer_3_out), .sel(nor_6_out));
  assign controlled_buffer_1_out = PCLK ? nor_1_out : 1'bz;  // Controlled_Buffer controlled_buffer_1
  assign controlled_buffer_2_out = PCLK ? nor_2_out : 1'bz;  // Controlled_Buffer controlled_buffer_2
  assign controlled_buffer_3_out = PCLK ? nor_3_out : 1'bz;  // Controlled_Buffer controlled_buffer_3
  assign controlled_buffer_1_out = LOAD ? IN0 : 1'bz;  // Controlled_Buffer controlled_buffer_4
  D_latch d_latch_1 (.EN(PCLK), .D(multiplexer_1_out), .NOT_Q(d_latch_1_not_q));  // open: Q
  assign controlled_buffer_1_out = STEP ? d_latch_1_not_q : 1'bz;  // Controlled_Buffer controlled_buffer_5
  assign controlled_buffer_2_out = LOAD ? IN1 : 1'bz;  // Controlled_Buffer controlled_buffer_6
  D_latch d_latch_2 (.EN(PCLK), .D(multiplexer_2_out), .NOT_Q(d_latch_2_not_q));  // open: Q
  assign controlled_buffer_2_out = STEP ? d_latch_2_not_q : 1'bz;  // Controlled_Buffer controlled_buffer_7
  assign controlled_buffer_3_out = LOAD ? IN2 : 1'bz;  // Controlled_Buffer controlled_buffer_8
  D_latch d_latch_3 (.EN(PCLK), .D(multiplexer_3_out), .NOT_Q(d_latch_3_not_q));  // open: Q
  assign controlled_buffer_3_out = STEP ? d_latch_3_not_q : 1'bz;  // Controlled_Buffer controlled_buffer_9
  nor nor_4 (TxZ, nQ2, nQ1, nQ0, BLNK, _111);
  D_latch d_latch_4 (.EN(1'b1), .D(controlled_buffer_1_out), .Q(Q0), .NOT_Q(nQ0));
  nor nor_5 (nor_5_out, nQ0, not_1_out);
  not not_1 (not_1_out, CARRY_IN);
  D_latch d_latch_5 (.EN(1'b1), .D(controlled_buffer_2_out), .Q(Q1), .NOT_Q(nQ1));
  nor nor_6 (nor_6_out, nQ1, not_2_out);
  not not_2 (not_2_out, nor_5_out);
  D_latch d_latch_6 (.EN(1'b1), .D(controlled_buffer_3_out), .Q(Q2), .NOT_Q(nQ2));
endmodule

module PATTERN_READOUT (
  input  PCLK,
  input  H2_prime,
  input  BLNK,
  input  H1_prime,
  input  PAR_O,
  input  F_NT,
  input  H0_prime_prime,
  input  SH2,
  input  FVO0,
  input  OV0,
  input  FVO1,
  input  OV1,
  input  FVO2,
  input  OV2,
  input  OV3,
  input  PD0,
  input  OB0,
  input  PD1,
  input  OB1,
  input  PD2,
  input  OB2,
  input  PD3,
  input  OB3,
  input  PD4,
  input  OB4,
  input  PD5,
  input  OB5,
  input  PD6,
  input  OB6,
  input  PD7,
  input  OB7,
  input  OBSEL,
  input  O8_16,
  input  BGBSEL,
  output PARR,
  output PAD0,
  output PAD1,
  output PAD2,
  output PAD3,
  output PAD4,
  output PAD5,
  output PAD6,
  output PAD7,
  output PAD8,
  output PAD9,
  output PAD10,
  output PAD11,
  output PAD12
);

  wire controlled_buffer_1_out, d_latch_1_q, d_latch_2_not_q, d_latch_3_not_q, d_latch_4_not_q,
       d_latch_5_not_q, d_latch_6_not_q, d_latch_7_not_q, d_latch_8_not_q, d_latch_9_not_q, d_latch_10_not_q,
       d_latch_11_not_q, d_latch_12_not_q, d_latch_13_not_q, d_latch_14_not_q, d_latch_15_not_q,
       d_latch_16_not_q, d_latch_17_not_q, d_latch_18_not_q, d_latch_19_not_q, d_latch_20_not_q,
       d_latch_21_not_q, d_latch_22_not_q, d_latch_23_not_q, d_latch_24_not_q, d_latch_25_not_q,
       d_latch_26_not_q, d_latch_27_not_q, d_latch_28_not_q, d_latch_29_not_q, d_latch_30_not_q,
       d_latch_31_not_q, d_latch_32_not_q, d_latch_33_not_q, d_latch_34_not_q, d_latch_35_not_q,
       multiplexer_1_out, multiplexer_2_out, multiplexer_3_out, multiplexer_4_out, multiplexer_5_out,
       multiplexer_6_out, multiplexer_7_out, multiplexer_8_out, multiplexer_9_out, multiplexer_10_out,
       multiplexer_11_out, multiplexer_12_out, multiplexer_13_out, multiplexer_14_out, multiplexer_15_out,
       multiplexer_16_out, multiplexer_17_out, multiplexer_18_out, nor_1_out, nor_3_out, nor_4_out,
       not_1_out, not_2_out, not_3_out, not_4_out, not_5_out, not_6_out, not_7_out, not_8_out, not_9_out,
       not_10_out, not_11_out, not_12_out, not_13_out, not_14_out, not_15_out, not_16_out, not_17_out,
       not_18_out, not_19_out, not_20_out;

  not not_1 (not_1_out, H0_prime_prime);
  not not_2 (not_2_out, PCLK);
  not not_3 (not_3_out, H2_prime);
  nor nor_1 (nor_1_out, F_NT, not_1_out);
  not not_4 (not_4_out, nor_1_out);
  D_latch d_latch_1 (.EN(not_2_out), .D(not_4_out), .Q(d_latch_1_q));  // open: NOT_Q
  not not_5 (not_5_out, PD0);
  not not_6 (not_6_out, PD1);
  not not_7 (not_7_out, PD2);
  not not_8 (not_8_out, PD3);
  not not_9 (not_9_out, PD4);
  not not_10 (not_10_out, PD5);
  not not_11 (not_11_out, PD6);
  not not_12 (not_12_out, PD7);
  nor nor_2 (PARR, not_3_out, BLNK);
  nor nor_3 (nor_3_out, not_2_out, d_latch_1_q);
  nor nor_4 (nor_4_out, not_2_out, SH2);
  assign controlled_buffer_1_out = nor_4_out ? OB7 : 1'bz;  // Controlled_Buffer controlled_buffer_1
  D_latch d_latch_2 (.EN(not_2_out), .D(not_5_out), .NOT_Q(d_latch_2_not_q));  // open: Q
  D_latch d_latch_3 (.EN(not_2_out), .D(not_6_out), .NOT_Q(d_latch_3_not_q));  // open: Q
  D_latch d_latch_4 (.EN(not_2_out), .D(not_7_out), .NOT_Q(d_latch_4_not_q));  // open: Q
  D_latch d_latch_5 (.EN(not_2_out), .D(not_8_out), .NOT_Q(d_latch_5_not_q));  // open: Q
  D_latch d_latch_6 (.EN(not_2_out), .D(not_9_out), .NOT_Q(d_latch_6_not_q));  // open: Q
  D_latch d_latch_7 (.EN(not_2_out), .D(not_10_out), .NOT_Q(d_latch_7_not_q));  // open: Q
  D_latch d_latch_8 (.EN(not_2_out), .D(not_11_out), .NOT_Q(d_latch_8_not_q));  // open: Q
  D_latch d_latch_9 (.EN(not_2_out), .D(not_12_out), .NOT_Q(d_latch_9_not_q));  // open: Q
  D_latch d_latch_10 (.EN(nor_3_out), .D(OV0), .NOT_Q(d_latch_10_not_q));  // open: Q
  D_latch d_latch_11 (.EN(nor_3_out), .D(OV1), .NOT_Q(d_latch_11_not_q));  // open: Q
  D_latch d_latch_12 (.EN(nor_3_out), .D(OV2), .NOT_Q(d_latch_12_not_q));  // open: Q
  D_latch d_latch_13 (.EN(nor_3_out), .D(OV3), .NOT_Q(d_latch_13_not_q));  // open: Q
  D_latch d_latch_14 (.EN(nor_3_out), .D(d_latch_2_not_q), .NOT_Q(d_latch_14_not_q));  // open: Q
  D_latch d_latch_15 (.EN(nor_3_out), .D(OB0), .NOT_Q(d_latch_15_not_q));  // open: Q
  D_latch d_latch_16 (.EN(nor_3_out), .D(d_latch_3_not_q), .NOT_Q(d_latch_16_not_q));  // open: Q
  D_latch d_latch_17 (.EN(nor_3_out), .D(OB1), .NOT_Q(d_latch_17_not_q));  // open: Q
  D_latch d_latch_18 (.EN(nor_3_out), .D(d_latch_4_not_q), .NOT_Q(d_latch_18_not_q));  // open: Q
  D_latch d_latch_19 (.EN(nor_3_out), .D(OB2), .NOT_Q(d_latch_19_not_q));  // open: Q
  D_latch d_latch_20 (.EN(nor_3_out), .D(d_latch_5_not_q), .NOT_Q(d_latch_20_not_q));  // open: Q
  D_latch d_latch_21 (.EN(nor_3_out), .D(OB3), .NOT_Q(d_latch_21_not_q));  // open: Q
  D_latch d_latch_22 (.EN(nor_3_out), .D(d_latch_6_not_q), .NOT_Q(d_latch_22_not_q));  // open: Q
  D_latch d_latch_23 (.EN(nor_3_out), .D(OB4), .NOT_Q(d_latch_23_not_q));  // open: Q
  D_latch d_latch_24 (.EN(nor_3_out), .D(d_latch_7_not_q), .NOT_Q(d_latch_24_not_q));  // open: Q
  D_latch d_latch_25 (.EN(nor_3_out), .D(OB5), .NOT_Q(d_latch_25_not_q));  // open: Q
  D_latch d_latch_26 (.EN(nor_3_out), .D(d_latch_8_not_q), .NOT_Q(d_latch_26_not_q));  // open: Q
  D_latch d_latch_27 (.EN(nor_3_out), .D(OB6), .NOT_Q(d_latch_27_not_q));  // open: Q
  D_latch d_latch_28 (.EN(nor_3_out), .D(d_latch_9_not_q), .NOT_Q(d_latch_28_not_q));  // open: Q
  D_latch d_latch_29 (.EN(nor_3_out), .D(OB7), .NOT_Q(d_latch_29_not_q));  // open: Q
  D_latch d_latch_30 (.EN(nor_3_out), .D(OB0), .NOT_Q(d_latch_30_not_q));  // open: Q
  D_latch d_latch_31 (.EN(not_2_out), .D(controlled_buffer_1_out), .NOT_Q(d_latch_31_not_q));  // open: Q
  D_latch d_latch_32 (.EN(not_2_out), .D(d_latch_10_not_q), .NOT_Q(d_latch_32_not_q));  // open: Q
  D_latch d_latch_33 (.EN(not_2_out), .D(d_latch_11_not_q), .NOT_Q(d_latch_33_not_q));  // open: Q
  D_latch d_latch_34 (.EN(not_2_out), .D(d_latch_12_not_q), .NOT_Q(d_latch_34_not_q));  // open: Q
  D_latch d_latch_35 (.EN(not_2_out), .D(d_latch_13_not_q), .NOT_Q(d_latch_35_not_q));  // open: Q
  not not_13 (not_13_out, d_latch_32_not_q);
  not not_14 (not_14_out, d_latch_33_not_q);
  not not_15 (not_15_out, d_latch_34_not_q);
  not not_16 (not_16_out, d_latch_35_not_q);
  not not_17 (not_17_out, multiplexer_4_out);
  Multiplexer #(.enable("false")) multiplexer_1 (
    .in0(d_latch_32_not_q), .in1(not_13_out), .out(multiplexer_1_out), .sel(d_latch_31_not_q));
  Multiplexer #(.enable("false")) multiplexer_2 (
    .in0(d_latch_33_not_q), .in1(not_14_out), .out(multiplexer_2_out), .sel(d_latch_31_not_q));
  Multiplexer #(.enable("false")) multiplexer_3 (
    .in0(d_latch_34_not_q), .in1(not_15_out), .out(multiplexer_3_out), .sel(d_latch_31_not_q));
  Multiplexer #(.enable("false")) multiplexer_4 (
    .in0(d_latch_35_not_q), .in1(not_16_out), .out(multiplexer_4_out), .sel(d_latch_31_not_q));
  Multiplexer #(.disabled(0), .enable("false")) multiplexer_5 (
    .in0(d_latch_15_not_q), .in1(not_17_out), .out(multiplexer_5_out), .sel(O8_16));
  Multiplexer #(.enable("false")) multiplexer_6 (
    .in0(OBSEL), .in1(d_latch_30_not_q), .out(multiplexer_6_out), .sel(O8_16));
  Multiplexer #(.enable("false")) multiplexer_7 (.in0(FVO0), .in1(not_18_out), .out(multiplexer_7_out), .sel(PAR_O));
  not not_18 (not_18_out, multiplexer_1_out);
  Multiplexer #(.enable("false")) multiplexer_8 (.in0(FVO1), .in1(not_19_out), .out(multiplexer_8_out), .sel(PAR_O));
  not not_19 (not_19_out, multiplexer_2_out);
  Multiplexer #(.enable("false")) multiplexer_9 (.in0(FVO2), .in1(not_20_out), .out(multiplexer_9_out), .sel(PAR_O));
  not not_20 (not_20_out, multiplexer_3_out);
  Multiplexer #(.enable("false")) multiplexer_10 (
    .in0(d_latch_14_not_q), .in1(multiplexer_5_out), .out(multiplexer_10_out), .sel(PAR_O));
  Multiplexer #(.enable("false")) multiplexer_11 (
    .in0(d_latch_16_not_q), .in1(d_latch_17_not_q), .out(multiplexer_11_out), .sel(PAR_O));
  Multiplexer #(.enable("false")) multiplexer_12 (
    .in0(d_latch_18_not_q), .in1(d_latch_19_not_q), .out(multiplexer_12_out), .sel(PAR_O));
  Multiplexer #(.enable("false")) multiplexer_13 (
    .in0(d_latch_20_not_q), .in1(d_latch_21_not_q), .out(multiplexer_13_out), .sel(PAR_O));
  Multiplexer #(.enable("false")) multiplexer_14 (
    .in0(d_latch_22_not_q), .in1(d_latch_23_not_q), .out(multiplexer_14_out), .sel(PAR_O));
  Multiplexer #(.enable("false")) multiplexer_15 (
    .in0(d_latch_24_not_q), .in1(d_latch_25_not_q), .out(multiplexer_15_out), .sel(PAR_O));
  Multiplexer #(.enable("false")) multiplexer_16 (
    .in0(d_latch_26_not_q), .in1(d_latch_27_not_q), .out(multiplexer_16_out), .sel(PAR_O));
  Multiplexer #(.enable("false")) multiplexer_17 (
    .in0(d_latch_28_not_q), .in1(d_latch_29_not_q), .out(multiplexer_17_out), .sel(PAR_O));
  Multiplexer #(.enable("false")) multiplexer_18 (
    .in0(BGBSEL), .in1(multiplexer_6_out), .out(multiplexer_18_out), .sel(PAR_O));
  D_latch d_latch_36 (.EN(not_2_out), .D(multiplexer_7_out), .Q(PAD0));  // open: NOT_Q
  D_latch d_latch_37 (.EN(not_2_out), .D(multiplexer_8_out), .Q(PAD1));  // open: NOT_Q
  D_latch d_latch_38 (.EN(not_2_out), .D(multiplexer_9_out), .Q(PAD2));  // open: NOT_Q
  not not_21 (PAD3, H1_prime);
  D_latch d_latch_39 (.EN(not_2_out), .D(multiplexer_10_out), .NOT_Q(PAD4));  // open: Q
  D_latch d_latch_40 (.EN(not_2_out), .D(multiplexer_11_out), .NOT_Q(PAD5));  // open: Q
  D_latch d_latch_41 (.EN(not_2_out), .D(multiplexer_12_out), .NOT_Q(PAD6));  // open: Q
  D_latch d_latch_42 (.EN(not_2_out), .D(multiplexer_13_out), .NOT_Q(PAD7));  // open: Q
  D_latch d_latch_43 (.EN(not_2_out), .D(multiplexer_14_out), .NOT_Q(PAD8));  // open: Q
  D_latch d_latch_44 (.EN(not_2_out), .D(multiplexer_15_out), .NOT_Q(PAD9));  // open: Q
  D_latch d_latch_45 (.EN(not_2_out), .D(multiplexer_16_out), .NOT_Q(PAD10));  // open: Q
  D_latch d_latch_46 (.EN(not_2_out), .D(multiplexer_17_out), .NOT_Q(PAD11));  // open: Q
  D_latch d_latch_47 (.EN(not_2_out), .D(multiplexer_18_out), .NOT_Q(PAD12));  // open: Q

  // Notes on the sheet:
  //   OB0
  //    номер знакогенератора для OB
  //   обычный / удвоенный размер спрайта
  //    номер знакогенератора для BG
  //   O
  //   /PCLK
  //   OBSEL
  //   08/16
  //   VDIR
  //   08/16
  //   BGSEL
  //   PAR/O
  //   PA0 - PA2 - номер строки тайла 
  //   PA4 - PA11 - номер тайла в знакогенераторе
  //   PA12 - номер знакогенератора для OB или BG
  //   A/B  байт строки тайла
endmodule

module COLOR_IO (
  input  PCLK,
  input  DB_CB,
  input  CB_DB,
  input  nBW,
  input  RAM_CB0,
  input  DB0,
  input  RAM_CB1,
  input  DB1,
  input  RAM_CB2,
  input  DB2,
  input  RAM_CB3,
  input  DB3,
  input  RAM_CB4,
  input  DB4,
  input  RAM_CB5,
  input  DB5,
  output nout0,
  output DB0_2,
  output CB_RAM0,
  output nout1,
  output DB1_2,
  output CB_RAM1,
  output nout2,
  output DB2_2,
  output CB_RAM2,
  output nout3,
  output DB3_2,
  output CB_RAM3,
  output nout4,
  output DB4_2,
  output CB_RAM4,
  output nout5,
  output DB5_2,
  output CB_RAM5
);

  wire _11_2_out, _11_3_out, _11_4_out, _11_5_out, _11_6_out, _11_out, d_ff_1_q, d_ff_2_q, d_ff_3_q,
       d_ff_4_q, d_ff_5_q, d_ff_6_q, d_latch_5_not_q, d_latch_6_not_q, d_latch_7_not_q, d_latch_8_not_q,
       d_latch_9_not_q, d_latch_10_not_q, d_latch_11_not_q, d_latch_12_not_q, d_latch_13_not_q,
       d_latch_14_not_q, d_latch_15_not_q, d_latch_16_not_q, d_latch_17_not_q, d_latch_18_not_q,
       d_latch_20_not_q, d_latch_22_not_q, nor_1_out, nor_2_out, nor_3_out, nor_4_out, nor_5_out, nor_6_out,
       not_1_out, not_2_out, not_3_out, not_4_out, not_5_out, not_6_out, not_7_out, not_8_out, not_9_out,
       not_10_out, not_11_out, not_12_out, not_13_out;

  D_Flip_Flop d_ff_1 (.clk(PCLK), .D(RAM_CB0), .Q(d_ff_1_q));  // open: Qn, preset, en, reset
  D_Flip_Flop d_ff_2 (.clk(PCLK), .D(RAM_CB1), .Q(d_ff_2_q));  // open: Qn, preset, en, reset
  D_Flip_Flop d_ff_3 (.clk(PCLK), .D(RAM_CB2), .Q(d_ff_3_q));  // open: Qn, preset, en, reset
  D_Flip_Flop d_ff_4 (.clk(PCLK), .D(RAM_CB3), .Q(d_ff_4_q));  // open: Qn, preset, en, reset
  D_Flip_Flop d_ff_5 (.clk(PCLK), .D(RAM_CB4), .Q(d_ff_5_q));  // open: Qn, preset, en, reset
  D_Flip_Flop d_ff_6 (.clk(PCLK), .D(RAM_CB5), .Q(d_ff_6_q));  // open: Qn, preset, en, reset
  nand _11 (_11_out, d_ff_1_q, nBW);
  nand _11_2 (_11_2_out, d_ff_2_q, nBW);
  nand _11_3 (_11_3_out, d_ff_3_q, nBW);
  nand _11_4 (_11_4_out, d_ff_4_q, nBW);
  nand _11_5 (_11_5_out, d_ff_5_q, 1'b1);
  nand _11_6 (_11_6_out, d_ff_6_q, 1'b1);
  not not_1 (not_1_out, PCLK);
  not not_2 (not_2_out, _11_out);
  not not_3 (not_3_out, DB0);
  not not_4 (not_4_out, _11_2_out);
  not not_5 (not_5_out, DB1);
  not not_6 (not_6_out, _11_3_out);
  not not_7 (not_7_out, DB2);
  not not_8 (not_8_out, _11_4_out);
  not not_9 (not_9_out, DB3);
  not not_10 (not_10_out, _11_5_out);
  not not_11 (not_11_out, DB4);
  not not_12 (not_12_out, _11_6_out);
  not not_13 (not_13_out, DB5);
  D_latch d_latch_1 (.EN(not_1_out), .D(not_2_out), .NOT_Q(nout0));  // open: Q
  D_latch d_latch_2 (.EN(not_1_out), .D(not_4_out), .NOT_Q(nout1));  // open: Q
  D_latch d_latch_3 (.EN(not_1_out), .D(not_6_out), .NOT_Q(nout2));  // open: Q
  D_latch d_latch_4 (.EN(not_1_out), .D(not_8_out), .NOT_Q(nout3));  // open: Q
  D_latch d_latch_5 (.EN(not_1_out), .D(not_10_out), .NOT_Q(d_latch_5_not_q));  // open: Q
  D_latch d_latch_6 (.EN(not_1_out), .D(not_12_out), .NOT_Q(d_latch_6_not_q));  // open: Q
  D_latch d_latch_7 (.EN(PCLK), .D(not_2_out), .NOT_Q(d_latch_7_not_q));  // open: Q
  D_latch d_latch_8 (.EN(PCLK), .D(not_4_out), .NOT_Q(d_latch_8_not_q));  // open: Q
  D_latch d_latch_9 (.EN(PCLK), .D(not_6_out), .NOT_Q(d_latch_9_not_q));  // open: Q
  D_latch d_latch_10 (.EN(PCLK), .D(not_8_out), .NOT_Q(d_latch_10_not_q));  // open: Q
  D_latch d_latch_11 (.EN(PCLK), .D(d_latch_5_not_q), .NOT_Q(d_latch_11_not_q));  // open: Q
  D_latch d_latch_12 (.EN(PCLK), .D(not_10_out), .NOT_Q(d_latch_12_not_q));  // open: Q
  D_latch d_latch_13 (.EN(PCLK), .D(d_latch_6_not_q), .NOT_Q(d_latch_13_not_q));  // open: Q
  D_latch d_latch_14 (.EN(PCLK), .D(not_12_out), .NOT_Q(d_latch_14_not_q));  // open: Q
  D_latch d_latch_15 (.EN(not_1_out), .D(d_latch_7_not_q), .NOT_Q(d_latch_15_not_q));  // open: Q
  D_latch d_latch_16 (.EN(not_1_out), .D(d_latch_8_not_q), .NOT_Q(d_latch_16_not_q));  // open: Q
  D_latch d_latch_17 (.EN(not_1_out), .D(d_latch_9_not_q), .NOT_Q(d_latch_17_not_q));  // open: Q
  D_latch d_latch_18 (.EN(not_1_out), .D(d_latch_10_not_q), .NOT_Q(d_latch_18_not_q));  // open: Q
  D_latch d_latch_19 (.EN(not_1_out), .D(d_latch_11_not_q), .NOT_Q(nout4));  // open: Q
  D_latch d_latch_20 (.EN(not_1_out), .D(d_latch_12_not_q), .NOT_Q(d_latch_20_not_q));  // open: Q
  D_latch d_latch_21 (.EN(not_1_out), .D(d_latch_13_not_q), .NOT_Q(nout5));  // open: Q
  D_latch d_latch_22 (.EN(not_1_out), .D(d_latch_14_not_q), .NOT_Q(d_latch_22_not_q));  // open: Q
  nor nor_1 (nor_1_out, d_latch_15_not_q, CB_DB);
  nor nor_2 (nor_2_out, d_latch_16_not_q, CB_DB);
  nor nor_3 (nor_3_out, d_latch_17_not_q, CB_DB);
  nor nor_4 (nor_4_out, d_latch_18_not_q, CB_DB);
  nor nor_5 (nor_5_out, d_latch_20_not_q, CB_DB);
  nor nor_6 (nor_6_out, d_latch_22_not_q, CB_DB);
  not not_14 (DB0_2, nor_1_out);
  nor nor_7 (CB_RAM0, DB_CB, not_3_out);
  not not_15 (DB1_2, nor_2_out);
  nor nor_8 (CB_RAM1, DB_CB, not_5_out);
  not not_16 (DB2_2, nor_3_out);
  nor nor_9 (CB_RAM2, DB_CB, not_7_out);
  not not_17 (DB3_2, nor_4_out);
  nor nor_10 (CB_RAM3, DB_CB, not_9_out);
  not not_18 (DB4_2, nor_5_out);
  nor nor_11 (CB_RAM4, DB_CB, not_11_out);
  not not_19 (DB5_2, nor_6_out);
  nor nor_12 (CB_RAM5, DB_CB, not_13_out);

  // Notes on the sheet:
  //   14
  //   6
  //   14
  //   6
  //   14
  //   6
  //   14
  //   6
  //   14
  //   6
  //   14
  //   6
  //   4
  //   4
  //   4
  //   4
  //   7
  //   4
  //   7
  //   4
  //   3
  //   3
  //   3
  //   3
  //   8
  //   3
  //   8
  //   3
endmodule

module WRITE__2007 (
  input  PCLK,
  input  DB_PAR,
  input  D0,
  input  D1,
  input  D2,
  input  D3,
  input  D4,
  input  D5,
  input  D6,
  input  D7,
  output PD0,
  output PD1,
  output PD2,
  output PD3,
  output PD4,
  output PD5,
  output PD6,
  output PD7
);

  wire d_latch_1_q, d_latch_2_q, d_latch_3_q, d_latch_4_q, d_latch_5_q, d_latch_6_q, d_latch_7_q, d_latch_8_q;

  D_latch d_latch_1 (.EN(PCLK), .D(D0), .Q(d_latch_1_q));  // open: NOT_Q
  D_latch d_latch_2 (.EN(PCLK), .D(D1), .Q(d_latch_2_q));  // open: NOT_Q
  D_latch d_latch_3 (.EN(PCLK), .D(D2), .Q(d_latch_3_q));  // open: NOT_Q
  D_latch d_latch_4 (.EN(PCLK), .D(D3), .Q(d_latch_4_q));  // open: NOT_Q
  D_latch d_latch_5 (.EN(PCLK), .D(D4), .Q(d_latch_5_q));  // open: NOT_Q
  D_latch d_latch_6 (.EN(PCLK), .D(D5), .Q(d_latch_6_q));  // open: NOT_Q
  D_latch d_latch_7 (.EN(PCLK), .D(D6), .Q(d_latch_7_q));  // open: NOT_Q
  D_latch d_latch_8 (.EN(PCLK), .D(D7), .Q(d_latch_8_q));  // open: NOT_Q
  assign PD0 = DB_PAR ? d_latch_1_q : 1'bz;  // Controlled_Buffer controlled_buffer_1
  assign PD1 = DB_PAR ? d_latch_2_q : 1'bz;  // Controlled_Buffer controlled_buffer_2
  assign PD2 = DB_PAR ? d_latch_3_q : 1'bz;  // Controlled_Buffer controlled_buffer_3
  assign PD3 = DB_PAR ? d_latch_4_q : 1'bz;  // Controlled_Buffer controlled_buffer_4
  assign PD4 = DB_PAR ? d_latch_5_q : 1'bz;  // Controlled_Buffer controlled_buffer_5
  assign PD5 = DB_PAR ? d_latch_6_q : 1'bz;  // Controlled_Buffer controlled_buffer_6
  assign PD6 = DB_PAR ? d_latch_7_q : 1'bz;  // Controlled_Buffer controlled_buffer_7
  assign PD7 = DB_PAR ? d_latch_8_q : 1'bz;  // Controlled_Buffer controlled_buffer_8
endmodule

// FIFO PIPELINE
module FIFO_PIPELINE (
  input  PCLK,
  input  T0,
  input  T1,
  input  T2,
  input  T3,
  input  T4,
  input  T5,
  input  T6,
  input  T7,
  input  SH7,
  input  SEL,
  input  SH5,
  input  SH3,
  input  SH2,
  input  _0_H,
  input  nVIS,
  input  OB0,
  input  OB1,
  input  OB2,
  input  OB3,
  input  OB4,
  input  OB5,
  input  OB6,
  input  OB7,
  output X_COL0,
  output X_COL1,
  output X_EN,
  output X_COL2,
  output X_COL3,
  output X_PRIO
);

  wire controlled_buffer_1_out, controlled_buffer_2_out, controlled_buffer_3_out, d_latch_1_not_q, nor_1_out,
       nor_2_out, nor_3_out, nor_4_out, nor_5_out, not_1_out;

  nor nor_1 (nor_1_out, not_1_out, d_latch_1_not_q, SH3);
  not not_1 (not_1_out, PCLK);
  FIFO_8BIT_COUNTER fifo_8bit_counter_1 (
    .PCLK(PCLK), ._0_H(_0_H), .nVIS(nVIS), .LOAD(nor_1_out), .IN0(OB0), .IN1(OB1), .IN2(OB2), .IN3(OB3),
    .IN4(OB4), .IN5(OB5), .IN6(OB6), .IN7(OB7), .X_EN(X_EN));
  D_latch d_latch_1 (.EN(not_1_out), .D(SEL), .NOT_Q(d_latch_1_not_q));  // open: Q
  nor nor_2 (nor_2_out, SH2, not_1_out, d_latch_1_not_q);
  assign controlled_buffer_1_out = nor_2_out ? OB0 : 1'bz;  // Controlled_Buffer controlled_buffer_1
  assign controlled_buffer_2_out = nor_2_out ? OB1 : 1'bz;  // Controlled_Buffer controlled_buffer_2
  assign controlled_buffer_3_out = nor_2_out ? OB5 : 1'bz;  // Controlled_Buffer controlled_buffer_3
  Pull_Resistor pull_resistor_1 (.node(controlled_buffer_1_out));
  Pull_Resistor pull_resistor_2 (.node(controlled_buffer_2_out));
  Pull_Resistor pull_resistor_3 (.node(controlled_buffer_3_out));
  nor nor_3 (nor_3_out, not_1_out, SH7, d_latch_1_not_q);
  nor nor_4 (nor_4_out, not_1_out, d_latch_1_not_q, SH5);
  nor nor_5 (nor_5_out, not_1_out, X_EN);
  D_latch d_latch_2 (.EN(not_1_out), .D(controlled_buffer_1_out), .Q(X_COL2));  // open: NOT_Q
  D_latch d_latch_3 (.EN(not_1_out), .D(controlled_buffer_2_out), .Q(X_COL3));  // open: NOT_Q
  D_latch d_latch_4 (.EN(not_1_out), .D(controlled_buffer_3_out), .Q(X_PRIO));  // open: NOT_Q
  SHIFT_REG_LOAD SHIFT_REGISTER_LOADABLE (
    .LOAD(nor_3_out), .STEP(nor_5_out), .NEXT(not_1_out), .OUT(X_COL0), ._0(T0), ._1(T1), ._2(T2), ._3(T3),
    ._4(T4), ._5(T5), ._6(T6), ._7(T7));
  SHIFT_REG_LOAD SHIFT_REGISTER_LOADABLE_2 (
    .LOAD(nor_4_out), .STEP(nor_5_out), .NEXT(not_1_out), .OUT(X_COL1), ._0(T0), ._1(T1), ._2(T2), ._3(T3),
    ._4(T4), ._5(T5), ._6(T6), ._7(T7));

  // Notes on the sheet:
  //   LOAD
  //   LDAT
  //   /PCLK
  //   T/SR0
  //   T/SR1
  //   /PCLK
  //   EN
endmodule

// FIFO_COUNTER
module FIFO_8BIT_COUNTER (
  input  PCLK,
  input  nVIS,
  input  _0_H,
  input  LOAD,
  input  IN0,
  input  IN1,
  input  IN2,
  input  IN3,
  input  IN4,
  input  IN5,
  input  IN6,
  input  IN7,
  output X_EN
);

  wire and_1_out, controlled_buffer_1_out, controlled_buffer_2_out, controlled_buffer_3_out,
       controlled_buffer_4_out, controlled_buffer_5_out, controlled_buffer_6_out, controlled_buffer_7_out,
       controlled_buffer_8_out, d_latch_1_not_q, d_latch_2_not_q, d_latch_3_not_q, d_latch_4_not_q,
       d_latch_5_not_q, d_latch_6_not_q, d_latch_7_not_q, d_latch_8_not_q, d_latch_10_not_q, d_latch_10_q,
       d_latch_11_not_q, d_latch_11_q, d_latch_12_not_q, d_latch_12_q, d_latch_13_not_q, d_latch_13_q,
       d_latch_14_not_q, d_latch_14_q, d_latch_15_not_q, d_latch_15_q, d_latch_16_not_q, d_latch_16_q,
       d_latch_17_not_q, d_latch_17_q, multiplexer_1_out, multiplexer_2_out, multiplexer_3_out,
       multiplexer_4_out, multiplexer_5_out, multiplexer_6_out, multiplexer_7_out, multiplexer_8_out,
       nor_1_out, nor_2_out, nor_3_out, nor_4_out, nor_5_out, nor_6_out, nor_7_out, nor_8_out, nor_9_out,
       nor_10_out, nor_11_out, nor_12_out, nor_13_out, nor_14_out, nor_15_out, not_1_out, not_2_out,
       not_3_out, not_4_out, not_5_out, not_6_out, not_7_out, not_8_out, not_9_out, not_10_out, not_11_out,
       not_12_out, not_13_out, not_14_out, not_15_out, not_16_out, not_17_out;

  nor nor_1 (nor_1_out, not_1_out, _0_H, nor_15_out);
  not not_1 (not_1_out, PCLK);
  nor nor_2 (nor_2_out, nor_1_out, nor_3_out);
  nor nor_3 (nor_3_out, nor_2_out, and_1_out);
  and and_1 (and_1_out, PCLK, nor_15_out);
  not not_2 (not_2_out, d_latch_10_not_q);
  not not_3 (not_3_out, d_latch_11_not_q);
  not not_4 (not_4_out, d_latch_12_not_q);
  not not_5 (not_5_out, d_latch_13_not_q);
  not not_6 (not_6_out, d_latch_14_not_q);
  not not_7 (not_7_out, d_latch_15_not_q);
  not not_8 (not_8_out, d_latch_16_not_q);
  not not_9 (not_9_out, d_latch_17_not_q);
  Multiplexer #(.enable("false")) multiplexer_1 (
    .in0(d_latch_10_not_q), .in1(not_2_out), .out(multiplexer_1_out), .sel(1'b1));
  Multiplexer #(.enable("false")) multiplexer_2 (
    .in0(d_latch_11_not_q), .in1(not_3_out), .out(multiplexer_2_out), .sel(nor_8_out));
  Multiplexer #(.enable("false")) multiplexer_3 (
    .in0(d_latch_12_not_q), .in1(not_4_out), .out(multiplexer_3_out), .sel(nor_9_out));
  Multiplexer #(.enable("false")) multiplexer_4 (
    .in0(d_latch_13_not_q), .in1(not_5_out), .out(multiplexer_4_out), .sel(nor_10_out));
  Multiplexer #(.enable("false")) multiplexer_5 (
    .in0(d_latch_14_not_q), .in1(not_6_out), .out(multiplexer_5_out), .sel(nor_11_out));
  Multiplexer #(.enable("false")) multiplexer_6 (
    .in0(d_latch_15_not_q), .in1(not_7_out), .out(multiplexer_6_out), .sel(nor_7_out));
  Multiplexer #(.enable("false")) multiplexer_7 (
    .in0(d_latch_16_not_q), .in1(not_8_out), .out(multiplexer_7_out), .sel(nor_13_out));
  Multiplexer #(.enable("false")) multiplexer_8 (
    .in0(d_latch_17_not_q), .in1(not_9_out), .out(multiplexer_8_out), .sel(nor_14_out));
  nor nor_4 (nor_4_out, PCLK, nor_2_out);
  nor nor_5 (nor_5_out, nor_4_out, LOAD);
  assign controlled_buffer_1_out = nor_5_out ? not_2_out : 1'bz;  // Controlled_Buffer controlled_buffer_1
  assign controlled_buffer_2_out = nor_5_out ? not_3_out : 1'bz;  // Controlled_Buffer controlled_buffer_2
  assign controlled_buffer_3_out = nor_5_out ? not_4_out : 1'bz;  // Controlled_Buffer controlled_buffer_3
  assign controlled_buffer_4_out = nor_5_out ? not_5_out : 1'bz;  // Controlled_Buffer controlled_buffer_4
  assign controlled_buffer_5_out = nor_5_out ? not_6_out : 1'bz;  // Controlled_Buffer controlled_buffer_5
  assign controlled_buffer_6_out = nor_5_out ? not_7_out : 1'bz;  // Controlled_Buffer controlled_buffer_6
  assign controlled_buffer_7_out = nor_5_out ? not_8_out : 1'bz;  // Controlled_Buffer controlled_buffer_7
  assign controlled_buffer_8_out = nor_5_out ? not_9_out : 1'bz;  // Controlled_Buffer controlled_buffer_8
  D_latch d_latch_1 (.EN(nor_5_out), .D(multiplexer_1_out), .NOT_Q(d_latch_1_not_q));  // open: Q
  D_latch d_latch_2 (.EN(nor_5_out), .D(multiplexer_2_out), .NOT_Q(d_latch_2_not_q));  // open: Q
  D_latch d_latch_3 (.EN(nor_5_out), .D(multiplexer_3_out), .NOT_Q(d_latch_3_not_q));  // open: Q
  D_latch d_latch_4 (.EN(nor_5_out), .D(multiplexer_4_out), .NOT_Q(d_latch_4_not_q));  // open: Q
  D_latch d_latch_5 (.EN(nor_5_out), .D(multiplexer_5_out), .NOT_Q(d_latch_5_not_q));  // open: Q
  D_latch d_latch_6 (.EN(nor_5_out), .D(multiplexer_6_out), .NOT_Q(d_latch_6_not_q));  // open: Q
  D_latch d_latch_7 (.EN(nor_5_out), .D(multiplexer_7_out), .NOT_Q(d_latch_7_not_q));  // open: Q
  D_latch d_latch_8 (.EN(nor_5_out), .D(multiplexer_8_out), .NOT_Q(d_latch_8_not_q));  // open: Q
  assign controlled_buffer_1_out = LOAD ? IN0 : 1'bz;  // Controlled_Buffer controlled_buffer_9
  assign controlled_buffer_1_out = nor_4_out ? d_latch_1_not_q : 1'bz;  // Controlled_Buffer controlled_buffer_10
  assign controlled_buffer_2_out = LOAD ? IN1 : 1'bz;  // Controlled_Buffer controlled_buffer_11
  assign controlled_buffer_2_out = nor_4_out ? d_latch_2_not_q : 1'bz;  // Controlled_Buffer controlled_buffer_12
  assign controlled_buffer_3_out = LOAD ? IN2 : 1'bz;  // Controlled_Buffer controlled_buffer_13
  assign controlled_buffer_3_out = nor_4_out ? d_latch_3_not_q : 1'bz;  // Controlled_Buffer controlled_buffer_14
  assign controlled_buffer_4_out = LOAD ? IN3 : 1'bz;  // Controlled_Buffer controlled_buffer_15
  assign controlled_buffer_4_out = nor_4_out ? d_latch_4_not_q : 1'bz;  // Controlled_Buffer controlled_buffer_16
  assign controlled_buffer_5_out = LOAD ? IN4 : 1'bz;  // Controlled_Buffer controlled_buffer_17
  assign controlled_buffer_5_out = nor_4_out ? d_latch_5_not_q : 1'bz;  // Controlled_Buffer controlled_buffer_18
  assign controlled_buffer_6_out = LOAD ? IN5 : 1'bz;  // Controlled_Buffer controlled_buffer_19
  assign controlled_buffer_6_out = nor_4_out ? d_latch_6_not_q : 1'bz;  // Controlled_Buffer controlled_buffer_20
  assign controlled_buffer_7_out = LOAD ? IN6 : 1'bz;  // Controlled_Buffer controlled_buffer_21
  assign controlled_buffer_7_out = nor_4_out ? d_latch_7_not_q : 1'bz;  // Controlled_Buffer controlled_buffer_22
  assign controlled_buffer_8_out = LOAD ? IN7 : 1'bz;  // Controlled_Buffer controlled_buffer_23
  assign controlled_buffer_8_out = nor_4_out ? d_latch_8_not_q : 1'bz;  // Controlled_Buffer controlled_buffer_24
  nor nor_6 (nor_6_out, nVIS, nor_3_out);
  not not_10 (not_10_out, 1'b1);
  not not_11 (not_11_out, nor_8_out);
  not not_12 (not_12_out, nor_9_out);
  not not_13 (not_13_out, nor_10_out);
  not not_14 (not_14_out, nor_11_out);
  nor nor_7 (nor_7_out, d_latch_14_q, d_latch_13_q, d_latch_12_q, d_latch_11_q, d_latch_10_q);
  not not_15 (not_15_out, nor_7_out);
  not not_16 (not_16_out, nor_13_out);
  not not_17 (not_17_out, nor_14_out);
  D_latch d_latch_9 (.EN(not_1_out), .D(nor_6_out), .NOT_Q(X_EN));  // open: Q
  D_latch d_latch_10 (.EN(1'b1), .D(controlled_buffer_1_out), .Q(d_latch_10_q), .NOT_Q(d_latch_10_not_q));
  nor nor_8 (nor_8_out, d_latch_10_not_q, not_10_out);
  D_latch d_latch_11 (.EN(1'b1), .D(controlled_buffer_2_out), .Q(d_latch_11_q), .NOT_Q(d_latch_11_not_q));
  nor nor_9 (nor_9_out, d_latch_11_not_q, not_11_out);
  D_latch d_latch_12 (.EN(1'b1), .D(controlled_buffer_3_out), .Q(d_latch_12_q), .NOT_Q(d_latch_12_not_q));
  nor nor_10 (nor_10_out, d_latch_12_not_q, not_12_out);
  D_latch d_latch_13 (.EN(1'b1), .D(controlled_buffer_4_out), .Q(d_latch_13_q), .NOT_Q(d_latch_13_not_q));
  nor nor_11 (nor_11_out, d_latch_13_not_q, not_13_out);
  D_latch d_latch_14 (.EN(1'b1), .D(controlled_buffer_5_out), .Q(d_latch_14_q), .NOT_Q(d_latch_14_not_q));
  nor nor_12 (nor_12_out, d_latch_14_not_q, not_14_out);
  D_latch d_latch_15 (.EN(1'b1), .D(controlled_buffer_6_out), .Q(d_latch_15_q), .NOT_Q(d_latch_15_not_q));
  nor nor_13 (nor_13_out, d_latch_15_not_q, not_15_out);
  D_latch d_latch_16 (.EN(1'b1), .D(controlled_buffer_7_out), .Q(d_latch_16_q), .NOT_Q(d_latch_16_not_q));
  nor nor_14 (nor_14_out, d_latch_16_not_q, not_16_out);
  D_latch d_latch_17 (.EN(1'b1), .D(controlled_buffer_8_out), .Q(d_latch_17_q), .NOT_Q(d_latch_17_not_q));
  nor nor_15 (nor_15_out, d_latch_17_not_q, not_17_out);

  // Notes on the sheet:
  //   UPD
  //   STEP
  //   LOAD
  //   CARRY OUT
endmodule

// SELECT PIXEL
module SELECT_EACH_2_3_5_7_PIX (
  input  PCLK,
  input  PAR_O,
  input  H0_prime_prime,
  input  H1_prime_prime,
  input  H2_prime_prime,
  output SH2,
  output SH3,
  output SH5,
  output SH7
);

  wire nor_1_out, nor_2_out, nor_3_out, nor_4_out, not_1_out, not_2_out, not_3_out, not_4_out, not_5_out;

  not not_1 (not_1_out, H2_prime_prime);
  not not_2 (not_2_out, PCLK);
  not not_3 (not_3_out, PAR_O);
  not not_4 (not_4_out, H1_prime_prime);
  not not_5 (not_5_out, H0_prime_prime);
  nor nor_1 (nor_1_out, not_3_out, H0_prime_prime, not_4_out, H2_prime_prime);
  nor nor_2 (nor_2_out, not_3_out, not_5_out, not_4_out, H2_prime_prime);
  nor nor_3 (nor_3_out, not_3_out, not_5_out, not_4_out, not_1_out);
  nor nor_4 (nor_4_out, not_3_out, not_5_out, H1_prime_prime, not_1_out);
  D_latch d_latch_1 (.EN(not_2_out), .D(nor_1_out), .NOT_Q(SH2));  // open: Q
  D_latch d_latch_2 (.EN(not_2_out), .D(nor_2_out), .NOT_Q(SH3));  // open: Q
  D_latch d_latch_3 (.EN(not_2_out), .D(nor_3_out), .NOT_Q(SH5));  // open: Q
  D_latch d_latch_4 (.EN(not_2_out), .D(nor_4_out), .NOT_Q(SH7));  // open: Q
endmodule

module OAM_SECOND_COUNTER (
  input  nPCLK,
  input  OSTEP,
  input  ORES,
  output nQ0,
  output nQ1,
  output nQ2,
  output nQ3,
  output nQ4,
  output CARRY_OUT
);

  wire d_ff_1_q, d_ff_1_qn, d_ff_2_q, d_ff_2_qn, d_ff_3_q, d_ff_3_qn, d_ff_4_q, d_ff_4_qn, d_ff_5_q,
       d_ff_5_qn, d_ff_6_qn, d_ff_7_qn, d_ff_8_qn, d_ff_9_qn, d_ff_10_qn, multiplexer_1_out,
       multiplexer_2_out, multiplexer_3_out, multiplexer_4_out, multiplexer_5_out, nor_1_out, nor_2_out,
       nor_3_out, nor_4_out, not_1_out, not_2_out, not_3_out, not_4_out, not_5_out;

  D_Flip_Flop d_ff_1 (.clk(OSTEP), .D(d_ff_6_qn), .Q(d_ff_1_q), .Qn(d_ff_1_qn), .reset(ORES));  // open: preset, en
  not not_1 (not_1_out, 1'b1);
  nor nor_1 (nor_1_out, d_ff_1_q, not_1_out);
  D_Flip_Flop d_ff_2 (.clk(OSTEP), .D(d_ff_7_qn), .Q(d_ff_2_q), .Qn(d_ff_2_qn), .reset(ORES));  // open: preset, en
  not not_2 (not_2_out, nor_1_out);
  nor nor_2 (nor_2_out, d_ff_2_q, not_2_out);
  D_Flip_Flop d_ff_3 (.clk(OSTEP), .D(d_ff_8_qn), .Q(d_ff_3_q), .Qn(d_ff_3_qn), .reset(ORES));  // open: preset, en
  not not_3 (not_3_out, nor_2_out);
  nor nor_3 (nor_3_out, d_ff_3_q, not_3_out);
  D_Flip_Flop d_ff_4 (.clk(OSTEP), .D(d_ff_9_qn), .Q(d_ff_4_q), .Qn(d_ff_4_qn), .reset(ORES));  // open: preset, en
  not not_4 (not_4_out, nor_3_out);
  nor nor_4 (nor_4_out, d_ff_4_q, not_4_out);
  D_Flip_Flop d_ff_5 (.clk(OSTEP), .D(d_ff_10_qn), .Q(d_ff_5_q), .Qn(d_ff_5_qn), .reset(ORES));  // open: preset, en
  not not_5 (not_5_out, nor_4_out);
  nor nor_5 (CARRY_OUT, d_ff_5_q, not_5_out);
  Multiplexer #(.enable("false")) multiplexer_1 (.in0(d_ff_1_qn), .in1(d_ff_1_q), .out(multiplexer_1_out), .sel(1'b1));
  Multiplexer #(.enable("false")) multiplexer_2 (
    .in0(d_ff_2_qn), .in1(d_ff_2_q), .out(multiplexer_2_out), .sel(nor_1_out));
  Multiplexer #(.enable("false")) multiplexer_3 (
    .in0(d_ff_3_qn), .in1(d_ff_3_q), .out(multiplexer_3_out), .sel(nor_2_out));
  Multiplexer #(.enable("false")) multiplexer_4 (
    .in0(d_ff_4_qn), .in1(d_ff_4_q), .out(multiplexer_4_out), .sel(nor_3_out));
  Multiplexer #(.enable("false")) multiplexer_5 (
    .in0(d_ff_5_qn), .in1(d_ff_5_q), .out(multiplexer_5_out), .sel(nor_4_out));
  D_Flip_Flop d_ff_6 (.clk(nPCLK), .D(multiplexer_1_out), .Q(nQ0), .Qn(d_ff_6_qn));  // open: preset, en, reset
  D_Flip_Flop d_ff_7 (.clk(nPCLK), .D(multiplexer_2_out), .Q(nQ1), .Qn(d_ff_7_qn));  // open: preset, en, reset
  D_Flip_Flop d_ff_8 (.clk(nPCLK), .D(multiplexer_3_out), .Q(nQ2), .Qn(d_ff_8_qn));  // open: preset, en, reset
  D_Flip_Flop d_ff_9 (.clk(nPCLK), .D(multiplexer_4_out), .Q(nQ3), .Qn(d_ff_9_qn));  // open: preset, en, reset
  D_Flip_Flop d_ff_10 (.clk(nPCLK), .D(multiplexer_5_out), .Q(nQ4), .Qn(d_ff_10_qn));  // open: preset, en, reset
endmodule

// H INVERSION
module H_INVERSION (
  input  PCLK,
  input  SH2,
  input  OB6,
  input  _0_FIFO,
  input  PD0,
  input  PD1,
  input  PD2,
  input  PD3,
  input  PD4,
  input  PD5,
  input  PD6,
  input  PD7,
  output T0,
  output T1,
  output T2,
  output T3,
  output T4,
  output T5,
  output T6,
  output T7
);

  wire d_latch_1_q, d_latch_2_q, d_latch_3_q, d_latch_4_q, d_latch_5_q, d_latch_6_q, d_latch_7_q,
       d_latch_8_q, multiplexer_1_out, multiplexer_2_out, multiplexer_3_out, multiplexer_4_out,
       multiplexer_5_out, multiplexer_6_out, multiplexer_7_out, multiplexer_8_out, multiplexer_9_out,
       nor_1_out, not_1_out, not_2_out, not_3_out;

  not not_1 (not_1_out, PCLK);
  nor nor_1 (nor_1_out, not_1_out, SH2);
  not not_2 (not_2_out, not_3_out);
  Multiplexer #(.disabled(0), .enable("false")) multiplexer_1 (
    .in0(not_2_out), .in1(OB6), .out(multiplexer_1_out), .sel(nor_1_out));
  Multiplexer #(.disabled(0), .enable("false")) multiplexer_2 (
    .in0(PD0), .in1(PD7), .out(multiplexer_2_out), .sel(not_2_out));
  Multiplexer #(.disabled(0), .enable("false")) multiplexer_3 (
    .in0(PD1), .in1(PD6), .out(multiplexer_3_out), .sel(not_2_out));
  Multiplexer #(.disabled(0), .enable("false")) multiplexer_4 (
    .in0(PD2), .in1(PD5), .out(multiplexer_4_out), .sel(not_2_out));
  Multiplexer #(.disabled(0), .enable("false")) multiplexer_5 (
    .in0(PD3), .in1(PD4), .out(multiplexer_5_out), .sel(not_2_out));
  Multiplexer #(.disabled(0), .enable("false")) multiplexer_6 (
    .in0(PD4), .in1(PD3), .out(multiplexer_6_out), .sel(not_2_out));
  Multiplexer #(.disabled(0), .enable("false")) multiplexer_7 (
    .in0(PD5), .in1(PD2), .out(multiplexer_7_out), .sel(not_2_out));
  Multiplexer #(.disabled(0), .enable("false")) multiplexer_8 (
    .in0(PD6), .in1(PD1), .out(multiplexer_8_out), .sel(not_2_out));
  Multiplexer #(.disabled(0), .enable("false")) multiplexer_9 (
    .in0(PD7), .in1(PD0), .out(multiplexer_9_out), .sel(not_2_out));
  not not_3 (not_3_out, multiplexer_1_out);
  D_latch d_latch_1 (.EN(not_1_out), .D(multiplexer_2_out), .Q(d_latch_1_q));  // open: NOT_Q
  D_latch d_latch_2 (.EN(not_1_out), .D(multiplexer_3_out), .Q(d_latch_2_q));  // open: NOT_Q
  D_latch d_latch_3 (.EN(not_1_out), .D(multiplexer_4_out), .Q(d_latch_3_q));  // open: NOT_Q
  D_latch d_latch_4 (.EN(not_1_out), .D(multiplexer_5_out), .Q(d_latch_4_q));  // open: NOT_Q
  D_latch d_latch_5 (.EN(not_1_out), .D(multiplexer_6_out), .Q(d_latch_5_q));  // open: NOT_Q
  D_latch d_latch_6 (.EN(not_1_out), .D(multiplexer_7_out), .Q(d_latch_6_q));  // open: NOT_Q
  D_latch d_latch_7 (.EN(not_1_out), .D(multiplexer_8_out), .Q(d_latch_7_q));  // open: NOT_Q
  D_latch d_latch_8 (.EN(not_1_out), .D(multiplexer_9_out), .Q(d_latch_8_q));  // open: NOT_Q
  nor nor_2 (T0, _0_FIFO, d_latch_1_q);
  nor nor_3 (T1, _0_FIFO, d_latch_2_q);
  nor nor_4 (T2, _0_FIFO, d_latch_3_q);
  nor nor_5 (T3, _0_FIFO, d_latch_4_q);
  nor nor_6 (T4, _0_FIFO, d_latch_5_q);
  nor nor_7 (T5, _0_FIFO, d_latch_6_q);
  nor nor_8 (T6, _0_FIFO, d_latch_7_q);
  nor nor_9 (T7, _0_FIFO, d_latch_8_q);

  // Notes on the sheet:
  //   HINV
endmodule

// OAM EVAL
module OAM_EVAL (
  input  PCLK,
  input  F_NT,
  input  H0_prime_prime,
  input  I_OAM2,
  input  nVIS,
  input  WTF,
  input  S_EV,
  input  PAR_O,
  input  O8_16,
  input  OB0,
  input  OB1,
  input  OB2,
  input  OB3,
  input  OB4,
  input  OB5,
  input  OB6,
  input  OB7,
  input  V0,
  input  V1,
  input  V2,
  input  V3,
  input  V4,
  input  V5,
  input  V6,
  input  V7,
  output _0_FIFO,
  output OMFG,
  output LOL,
  output OV0,
  output OV1,
  output OV2,
  output OV3
);

  wire _2_out, _3_out, _10_out, _14_out, _18_out, _19_out, _20_out, _24_out, _29_out, and_1_out, and_2_out,
       and_3_out, d_latch_1_not_q, d_latch_2_not_q, d_latch_3_q, d_latch_4_not_q, d_latch_5_not_q,
       d_latch_6_not_q, d_latch_7_not_q, d_latch_8_not_q, d_latch_9_not_q, multiplexer_1_out,
       multiplexer_2_out, multiplexer_3_out, nor_1_out, not_1_out, not_2_out, not_3_out, not_4_out,
       not_6_out, not_7_out, not_8_out, not_9_out, not_12_out, not_13_out, not_14_out, nPCLK, oam_sub_1_ov4,
       oam_sub_1_ov5, oam_sub_1_ov6, oam_sub_1_ov7;

  not not_1 (not_1_out, H0_prime_prime);
  not not_2 (not_2_out, S_EV);
  not not_3 (not_3_out, PAR_O);
  not not_4 (not_4_out, O8_16);
  not not_5 (nPCLK, PCLK);
  nor _29 (_29_out, I_OAM2, nVIS, WTF, not_14_out);
  nor _20 (_20_out, F_NT, not_1_out);
  nor _19 (_19_out, PCLK, not_1_out);
  and and_1 (and_1_out, _29_out, _24_out);
  nor _24 (_24_out, not_2_out, PCLK);
  nor _2 (_2_out, PCLK, not_3_out);
  not not_6 (not_6_out, _20_out);
  D_latch d_latch_1 (.EN(_19_out), .D(_29_out), .NOT_Q(d_latch_1_not_q));  // open: Q
  OAM_SUB oam_sub_1 (
    .PCLK(PCLK), .OB0(OB0), .OB1(OB1), .OB2(OB2), .OB3(OB3), .OB4(OB4), .OB5(OB5), .OB6(OB6), .OB7(OB7),
    .V0(V0), .V1(V1), .V2(V2), .V3(V3), .V4(V4), .V5(V5), .V6(V6), .V7(V7), .OV0(OV0), .OV1(OV1), .OV2(OV2),
    .OV3(OV3), .OV4(oam_sub_1_ov4), .OV5(oam_sub_1_ov5), .OV6(oam_sub_1_ov6), .OV7(oam_sub_1_ov7));
  D_latch d_latch_2 (.EN(PCLK), .D(OB7), .NOT_Q(d_latch_2_not_q));  // open: Q
  D_latch d_latch_3 (.EN(nPCLK), .D(not_6_out), .Q(d_latch_3_q));  // open: NOT_Q
  D_latch d_latch_4 (.EN(PCLK), .D(d_latch_1_not_q), .NOT_Q(d_latch_4_not_q));  // open: Q
  not not_7 (not_7_out, multiplexer_1_out);
  Multiplexer #(.disabled(0), .enable("false")) multiplexer_1 (
    .in0(not_8_out), .in1(and_1_out), .out(multiplexer_1_out), .sel(PCLK));
  not not_8 (not_8_out, not_7_out);
  nor _14 (_14_out, d_latch_2_not_q, V7);
  nor _18 (_18_out, nPCLK, d_latch_3_q);
  D_latch d_latch_5 (.EN(_19_out), .D(d_latch_4_not_q), .NOT_Q(d_latch_5_not_q));  // open: Q
  D_latch d_latch_6 (.EN(PCLK), .D(d_latch_5_not_q), .NOT_Q(d_latch_6_not_q));  // open: Q
  Multiplexer #(.disabled(0), .enable("false")) multiplexer_2 (
    .in0(LOL), .in1(and_2_out), .out(multiplexer_2_out), .sel(PCLK));
  and and_2 (and_2_out, not_8_out, _2_out);
  D_latch d_latch_7 (.EN(nPCLK), .D(not_14_out), .NOT_Q(d_latch_7_not_q));  // open: Q
  and and_3 (and_3_out, d_latch_7_not_q, _18_out);
  D_latch d_latch_8 (.EN(_19_out), .D(d_latch_6_not_q), .NOT_Q(d_latch_8_not_q));  // open: Q
  not not_9 (not_9_out, multiplexer_2_out);
  not not_10 (LOL, not_9_out);
  Multiplexer #(.disabled(0), .enable("false")) multiplexer_3 (
    .in0(_0_FIFO), .in1(and_3_out), .out(multiplexer_3_out), .sel(nPCLK));
  not not_11 (_0_FIFO, not_12_out);
  D_latch d_latch_9 (.EN(PCLK), .D(d_latch_8_not_q), .NOT_Q(d_latch_9_not_q));  // open: Q
  and _3 (_3_out, not_4_out, OV3);
  not not_12 (not_12_out, multiplexer_3_out);
  not not_13 (not_13_out, _10_out);
  nor _10 (_10_out, d_latch_9_not_q, d_latch_6_not_q, d_latch_4_not_q);
  not not_14 (not_14_out, nor_1_out);
  nor nor_1 (nor_1_out, not_13_out, _3_out, oam_sub_1_ov4, oam_sub_1_ov5, oam_sub_1_ov6, oam_sub_1_ov7, _14_out);
  nor _12 (OMFG, not_13_out, _29_out);

  // Notes on the sheet:
  //   22
  //   23
  //   1
  //   3
  //   /I2
  //   21
  //   DDD
  //   1
  //   9
  //   2
  //   FF2
  //   9
  //   3
  //   4
  //   8
  //   5
  //   FF1
  //   LOL
  //   6
  //   FF3
  //   11
  //   OVZ
  //   29
endmodule

// OAM BUF CONTROL
module OAM_BUF_CONTROL (
  input  PCLK,
  input  BLNK,
  input  WTF,
  input  nVIS,
  input  MILF,
  input  H0_prime_prime,
  input  nW4,
  input  nDBE,
  output DB_OB,
  output nOE,
  output OFETCH
);

  wire _1_out, _4_out, _6_out, _8_out, _9_out, and_1_out, d_latch_1_not_q, d_latch_2_not_q, d_latch_3_not_q,
       d_latch_4_q, multiplexer_1_out, not_1_out, not_2_out, not_3_out, not_4_out;

  not not_1 (not_1_out, H0_prime_prime);
  not not_2 (not_2_out, PCLK);
  nor _1 (_1_out, nW4, nDBE);
  nor _7 (DB_OB, not_2_out, BLNK);
  nor _4 (_4_out, BLNK, PCLK, WTF, nVIS, MILF, not_1_out);
  nor _8 (_8_out, _1_out, _9_out);
  nor _9 (_9_out, _8_out, d_latch_3_not_q);
  nor _6 (_6_out, _1_out, _8_out);
  and and_1 (and_1_out, PCLK, _6_out);
  Multiplexer #(.disabled(0), .enable("false")) multiplexer_1 (
    .in0(and_1_out), .in1(not_4_out), .out(multiplexer_1_out), .sel(not_2_out));
  not not_3 (not_3_out, multiplexer_1_out);
  not not_4 (not_4_out, not_3_out);
  D_latch d_latch_1 (.EN(not_2_out), .D(not_3_out), .NOT_Q(d_latch_1_not_q));  // open: Q
  D_latch d_latch_2 (.EN(PCLK), .D(d_latch_1_not_q), .NOT_Q(d_latch_2_not_q));  // open: Q
  D_latch d_latch_3 (.EN(not_2_out), .D(d_latch_2_not_q), .NOT_Q(d_latch_3_not_q));  // open: Q
  D_latch d_latch_4 (.EN(PCLK), .D(d_latch_3_not_q), .Q(d_latch_4_q));  // open: NOT_Q
  nor _3 (nOE, _4_out, OFETCH);
  nor _10 (OFETCH, d_latch_4_q, d_latch_2_not_q);

  // Notes on the sheet:
  //   5
  //   FF1
  //   FF2
  //   1
  //   2
  //   3
  //   4
endmodule
module SHIFT_REG (
  input  STEP1,
  input  DATA_IN,
  input  STEP2,
  output OUT_0,
  output OUT_1,
  output OUT_2,
  output OUT_3,
  output OUT_4,
  output OUT_5,
  output OUT_6,
  output OUT_7
);

  wire d_latch_1_not_q, d_latch_3_not_q, d_latch_5_not_q, d_latch_7_not_q, d_latch_9_not_q, d_latch_11_not_q,
       d_latch_13_not_q, d_latch_15_not_q;

  D_latch d_latch_1 (.EN(STEP1), .D(DATA_IN), .NOT_Q(d_latch_1_not_q));  // open: Q
  D_latch d_latch_2 (.EN(STEP2), .D(d_latch_1_not_q), .NOT_Q(OUT_0));  // open: Q
  D_latch d_latch_3 (.EN(STEP1), .D(OUT_0), .NOT_Q(d_latch_3_not_q));  // open: Q
  D_latch d_latch_4 (.EN(STEP2), .D(d_latch_3_not_q), .NOT_Q(OUT_1));  // open: Q
  D_latch d_latch_5 (.EN(STEP1), .D(OUT_1), .NOT_Q(d_latch_5_not_q));  // open: Q
  D_latch d_latch_6 (.EN(STEP2), .D(d_latch_5_not_q), .NOT_Q(OUT_2));  // open: Q
  D_latch d_latch_7 (.EN(STEP1), .D(OUT_2), .NOT_Q(d_latch_7_not_q));  // open: Q
  D_latch d_latch_8 (.EN(STEP2), .D(d_latch_7_not_q), .NOT_Q(OUT_3));  // open: Q
  D_latch d_latch_9 (.EN(STEP1), .D(OUT_3), .NOT_Q(d_latch_9_not_q));  // open: Q
  D_latch d_latch_10 (.EN(STEP2), .D(d_latch_9_not_q), .NOT_Q(OUT_4));  // open: Q
  D_latch d_latch_11 (.EN(STEP1), .D(OUT_4), .NOT_Q(d_latch_11_not_q));  // open: Q
  D_latch d_latch_12 (.EN(STEP2), .D(d_latch_11_not_q), .NOT_Q(OUT_5));  // open: Q
  D_latch d_latch_13 (.EN(STEP1), .D(OUT_5), .NOT_Q(d_latch_13_not_q));  // open: Q
  D_latch d_latch_14 (.EN(STEP2), .D(d_latch_13_not_q), .NOT_Q(OUT_6));  // open: Q
  D_latch d_latch_15 (.EN(STEP1), .D(OUT_6), .NOT_Q(d_latch_15_not_q));  // open: Q
  D_latch d_latch_16 (.EN(STEP2), .D(d_latch_15_not_q), .NOT_Q(OUT_7));  // open: Q
endmodule

module SEL_1_8 (
  input  _0,
  input  _1,
  input  _2,
  input  _3,
  input  _4,
  input  _5,
  input  _6,
  input  _7,
  input  FH0,
  input  FH1,
  input  FH2,
  output OUT
);

  wire and_1_out, and_2_out, and_3_out, and_4_out, and_5_out, and_6_out, and_7_out, and_8_out, not_1_out,
       not_2_out, not_3_out;

  not not_1 (not_1_out, FH0);
  not not_2 (not_2_out, FH1);
  not not_3 (not_3_out, FH2);
  and and_1 (and_1_out, FH2, FH1, FH0, _0);
  and and_2 (and_2_out, FH2, FH1, not_1_out, _1);
  and and_3 (and_3_out, FH2, not_2_out, FH0, _2);
  and and_4 (and_4_out, FH2, not_2_out, not_1_out, _3);
  and and_5 (and_5_out, not_3_out, FH1, FH0, _4);
  and and_6 (and_6_out, not_3_out, FH1, not_1_out, _5);
  and and_7 (and_7_out, not_3_out, not_2_out, FH0, _6);
  and and_8 (and_8_out, not_3_out, not_2_out, not_1_out, _7);
  or or_1 (OUT, and_8_out, and_7_out, and_6_out, and_5_out, and_4_out, and_3_out, and_2_out, and_1_out);
endmodule

module SEL_1_4 (
  input  _0,
  input  _1,
  input  _2,
  input  _3,
  input  HO1,
  input  VO1,
  output OUT
);

  wire and_1_out, and_2_out, and_3_out, and_4_out, not_1_out, not_2_out;

  not not_1 (not_1_out, HO1);
  not not_2 (not_2_out, VO1);
  and and_1 (and_1_out, VO1, HO1, _0);
  and and_2 (and_2_out, not_2_out, HO1, _2);
  and and_3 (and_3_out, VO1, not_1_out, _1);
  and and_4 (and_4_out, not_2_out, not_1_out, _3);
  or or_1 (OUT, and_4_out, and_2_out, and_3_out, and_1_out);
endmodule

module SHIFT_REG_LOAD (
  input  _0,
  input  _1,
  input  _2,
  input  _3,
  input  _4,
  input  _5,
  input  _6,
  input  _7,
  input  LOAD,
  input  STEP,
  input  NEXT,
  output OUT
);

  wire controlled_buffer_1_out, controlled_buffer_3_out, controlled_buffer_5_out, controlled_buffer_7_out,
       controlled_buffer_9_out, controlled_buffer_11_out, controlled_buffer_13_out, controlled_buffer_15_out,
       d_latch_1_not_q, d_latch_2_not_q, d_latch_3_not_q, d_latch_4_not_q, d_latch_5_not_q, d_latch_6_not_q,
       d_latch_7_not_q, d_latch_8_not_q, d_latch_9_not_q, d_latch_10_not_q, d_latch_11_not_q,
       d_latch_12_not_q, d_latch_13_not_q, d_latch_14_not_q, d_latch_15_not_q;

  assign controlled_buffer_1_out = STEP ? 1'b1 : 1'bz;  // Controlled_Buffer controlled_buffer_1
  assign controlled_buffer_1_out = LOAD ? _0 : 1'bz;  // Controlled_Buffer controlled_buffer_2
  D_latch d_latch_1 (.EN(1'b1), .D(controlled_buffer_1_out), .NOT_Q(d_latch_1_not_q));  // open: Q
  D_latch d_latch_2 (.EN(NEXT), .D(d_latch_1_not_q), .NOT_Q(d_latch_2_not_q));  // open: Q
  assign controlled_buffer_3_out = LOAD ? _1 : 1'bz;  // Controlled_Buffer controlled_buffer_3
  assign controlled_buffer_3_out = STEP ? d_latch_2_not_q : 1'bz;  // Controlled_Buffer controlled_buffer_4
  D_latch d_latch_3 (.EN(1'b1), .D(controlled_buffer_3_out), .NOT_Q(d_latch_3_not_q));  // open: Q
  D_latch d_latch_4 (.EN(NEXT), .D(d_latch_3_not_q), .NOT_Q(d_latch_4_not_q));  // open: Q
  assign controlled_buffer_5_out = STEP ? d_latch_4_not_q : 1'bz;  // Controlled_Buffer controlled_buffer_5
  assign controlled_buffer_5_out = LOAD ? _2 : 1'bz;  // Controlled_Buffer controlled_buffer_6
  D_latch d_latch_5 (.EN(1'b1), .D(controlled_buffer_5_out), .NOT_Q(d_latch_5_not_q));  // open: Q
  D_latch d_latch_6 (.EN(NEXT), .D(d_latch_5_not_q), .NOT_Q(d_latch_6_not_q));  // open: Q
  assign controlled_buffer_7_out = LOAD ? _3 : 1'bz;  // Controlled_Buffer controlled_buffer_7
  assign controlled_buffer_7_out = STEP ? d_latch_6_not_q : 1'bz;  // Controlled_Buffer controlled_buffer_8
  D_latch d_latch_7 (.EN(1'b1), .D(controlled_buffer_7_out), .NOT_Q(d_latch_7_not_q));  // open: Q
  D_latch d_latch_8 (.EN(NEXT), .D(d_latch_7_not_q), .NOT_Q(d_latch_8_not_q));  // open: Q
  assign controlled_buffer_9_out = STEP ? d_latch_8_not_q : 1'bz;  // Controlled_Buffer controlled_buffer_9
  assign controlled_buffer_9_out = LOAD ? _4 : 1'bz;  // Controlled_Buffer controlled_buffer_10
  D_latch d_latch_9 (.EN(1'b1), .D(controlled_buffer_9_out), .NOT_Q(d_latch_9_not_q));  // open: Q
  D_latch d_latch_10 (.EN(NEXT), .D(d_latch_9_not_q), .NOT_Q(d_latch_10_not_q));  // open: Q
  assign controlled_buffer_11_out = LOAD ? _5 : 1'bz;  // Controlled_Buffer controlled_buffer_11
  assign controlled_buffer_11_out = STEP ? d_latch_10_not_q : 1'bz;  // Controlled_Buffer controlled_buffer_12
  D_latch d_latch_11 (.EN(1'b1), .D(controlled_buffer_11_out), .NOT_Q(d_latch_11_not_q));  // open: Q
  D_latch d_latch_12 (.EN(NEXT), .D(d_latch_11_not_q), .NOT_Q(d_latch_12_not_q));  // open: Q
  assign controlled_buffer_13_out = STEP ? d_latch_12_not_q : 1'bz;  // Controlled_Buffer controlled_buffer_13
  assign controlled_buffer_13_out = LOAD ? _6 : 1'bz;  // Controlled_Buffer controlled_buffer_14
  D_latch d_latch_13 (.EN(1'b1), .D(controlled_buffer_13_out), .NOT_Q(d_latch_13_not_q));  // open: Q
  D_latch d_latch_14 (.EN(NEXT), .D(d_latch_13_not_q), .NOT_Q(d_latch_14_not_q));  // open: Q
  assign controlled_buffer_15_out = LOAD ? _7 : 1'bz;  // Controlled_Buffer controlled_buffer_15
  assign controlled_buffer_15_out = STEP ? d_latch_14_not_q : 1'bz;  // Controlled_Buffer controlled_buffer_16
  D_latch d_latch_15 (.EN(1'b1), .D(controlled_buffer_15_out), .NOT_Q(d_latch_15_not_q));  // open: Q
  D_latch d_latch_16 (.EN(NEXT), .D(d_latch_15_not_q), .NOT_Q(OUT));  // open: Q
endmodule
