// Logisim project CounterStage.circ as structural Verilog: 3 circuits, main circuit main
module main (
  input  CLR,
  input  CLK,
  input  carry_in,
  input  RES,
  output out,
  output carry_out
);

  wire DLatch_q, multiplexer_1_out, multiplexer_2_out, nor_3_out, not_1_out, not_2_out, not_3_out;

  not not_1 (not_1_out, CLK);
  Multiplexer multiplexer_1 (.in0(not_2_out), .in1(out), .out(multiplexer_1_out), .sel(carry_in));  // open: en
  not not_2 (not_2_out, multiplexer_2_out);
  Multiplexer multiplexer_2 (.in0(out), .in1(nor_3_out), .out(multiplexer_2_out), .sel(CLK));  // open: en
  not not_3 (not_3_out, carry_in);
  nor nor_1 (out, not_2_out, RES);
  nor nor_2 (carry_out, not_2_out, not_3_out);
  nor nor_3 (nor_3_out, DLatch_q, CLR);
  DLatch DLatch (.EN(not_1_out), .D(multiplexer_1_out), .Q(DLatch_q));  // open: NOT_Q

  // Notes on the sheet:
  //   clear manually
  //   global RESET
  //   FF
endmodule

module DLatch (
  input  EN,
  input  D,
  output Q,
  output NOT_Q
);

  D_Flip_Flop #(.trigger("high")) d_ff_1 (.clk(EN), .D(D), .Q(Q), .Qn(NOT_Q));  // open: preset, en, reset
endmodule

module _2BitCounter (
  input  CLR,
  input  RES,
  input  Carry_In,
  output Bit_0,
  output Bit_1
);

  wire main_1_carry_out, PCLK_out;

  Clock PCLK (.out(PCLK_out));
  main main_1 (.CLR(CLR), .CLK(PCLK_out), .carry_in(Carry_In), .RES(RES), .out(Bit_0), .carry_out(main_1_carry_out));
  main main_2 (.CLR(CLR), .CLK(PCLK_out), .carry_in(main_1_carry_out), .RES(RES), .out(Bit_1));  // open: carry_out
endmodule
