// Logisim project HV_FSM_Standalone_Evo.circ as structural Verilog
module HV_FSM (
);

  DelayedH DelayedH_inst ();  // open: H5_DashDash, H4_DashDash, H3_DashDash, H2_DashDash, n_H2_Dash, H1_DashDash, n_H1_Dash, H0_DashDash, H0_Dash, PCLK, n_PCLK, H_Input
endmodule

module DLatch (
  input  Enable,
  input  Value,
  output ValOut,
  output n_ValOut
);

  D_Flip_Flop #(.trigger("high")) d_ff_1 (.D(Value), .clk(Enable), .Q(ValOut), .Qn(n_ValOut));  // open: preset, reset
endmodule

module DelayedH (
  input  PCLK,
  input  n_PCLK,
  input  [8:0] H_Input,
  output H5_DashDash,
  output H4_DashDash,
  output H3_DashDash,
  output H2_DashDash,
  output n_H2_Dash,
  output H1_DashDash,
  output n_H1_Dash,
  output H0_DashDash,
  output H0_Dash
);

  wire h0_latch1_n_valout, h0_latch2_n_valout, h2_latch1_n_valout, h3_latch1_n_valout, h4_latch1_n_valout,
       h5_latch1_n_valout;

  DLatch h5_latch1 (.n_ValOut(h5_latch1_n_valout), .Enable(n_PCLK), .Value(H_Input[5]));  // open: ValOut
  DLatch h4_latch1 (.n_ValOut(h4_latch1_n_valout), .Enable(n_PCLK), .Value(H_Input[4]));  // open: ValOut
  DLatch h3_latch1 (.n_ValOut(h3_latch1_n_valout), .Enable(n_PCLK), .Value(H_Input[3]));  // open: ValOut
  DLatch h2_latch1 (.n_ValOut(h2_latch1_n_valout), .Enable(n_PCLK), .Value(H_Input[2]));  // open: ValOut
  DLatch h1_latch1 (.n_ValOut(n_H1_Dash), .Enable(n_PCLK), .Value(H_Input[1]));  // open: ValOut
  DLatch h0_latch1 (.n_ValOut(h0_latch1_n_valout), .Enable(n_PCLK), .Value(H_Input[0]));  // open: ValOut
  DLatch h5_latch2 (.n_ValOut(H5_DashDash), .Enable(PCLK), .Value(h5_latch1_n_valout));  // open: ValOut
  DLatch h4_latch2 (.n_ValOut(H4_DashDash), .Enable(PCLK), .Value(h4_latch1_n_valout));  // open: ValOut
  DLatch h3_latch2 (.n_ValOut(H3_DashDash), .Enable(PCLK), .Value(h3_latch1_n_valout));  // open: ValOut
  DLatch h2_latch2 (.n_ValOut(H2_DashDash), .Enable(PCLK), .Value(h2_latch1_n_valout));  // open: ValOut
  DLatch h1_latch2 (.n_ValOut(H1_DashDash), .Enable(PCLK), .Value(n_H1_Dash));  // open: ValOut
  DLatch h0_latch2 (.n_ValOut(h0_latch2_n_valout), .Enable(PCLK), .Value(h0_latch1_n_valout));  // open: ValOut
  buf buffer_1 (n_H2_Dash, h2_latch1_n_valout);
  buf buffer_2 (H0_DashDash, h0_latch2_n_valout);
  not not_1 (H0_Dash, h0_latch1_n_valout);
endmodule
