// Logisim project APUPlayer.circ as structural Verilog: 7 circuits, main circuit APUPlayer
module APUPlayer (
  input  nRES
);

  wire apu_dmc, apu_dmc_enirq, apu_dmc_loop, apu_nirq_cpu, apu_nnmi_cpu, apu_phi0__cpu, apu_r_w__ext,
       apu_rdy__cpu, apu_rmode, apu_rnd, apu_sqa, apu_sqb, apu_tri, core_phi1, core_phi2, core_r_w,
       Next_RegOp_out, XTAL_out;
  wire [1:0] apu_sqa_duty, apu_sqb_duty;
  wire [3:0] apu_dmcf, apu_n_req, transp_latch_q_2, transp_latch_q_3;
  wire [5:0] apu_n_env, apu_sqa_env, apu_sqb_env;
  wire [7:0] apu_aux_a, apu_data_to_cpu, apu_db_out_ext, apu_sample_adr, apu_sample_buf, apu_sample_length,
       apu_sw_a, apu_sw_b, apu_tri_lin, transp_latch_q, wram_db_out;
  wire [10:0] apu_sqa_f, apu_sqb_f, apu_tri_freq;
  wire [14:0] apu_aux_b;
  wire [15:0] apu_ab, core_addr;
  wire [23:0] dumper_addr;
  wire [31:0] core_out_15, dumper_data;

  Clock XTAL (.out(XTAL_out));
  LED DMC (.in(apu_dmc));
  LED TRI (.in(apu_tri));
  LED SQB (.in(apu_sqb));
  LED SQA (.in(apu_sqa));
  LED RND (.in(apu_rnd));
  LED led_1 (.in(apu_tri_freq[0]));
  LED led_2 (.in(apu_tri_freq[1]));
  LED led_3 (.in(apu_tri_freq[2]));
  LED led_4 (.in(apu_tri_freq[3]));
  LED led_5 (.in(apu_tri_freq[4]));
  LED led_6 (.in(apu_tri_freq[5]));
  LED led_7 (.in(apu_tri_freq[6]));
  LED led_8 (.in(apu_tri_freq[7]));
  LED led_9 (.in(apu_tri_freq[8]));
  LED led_10 (.in(apu_tri_freq[9]));
  LED led_11 (.in(apu_tri_freq[10]));
  LED led_12 (.in(apu_tri_lin[0]));
  LED led_13 (.in(apu_tri_lin[1]));
  LED led_14 (.in(apu_tri_lin[2]));
  LED led_15 (.in(apu_tri_lin[3]));
  LED led_16 (.in(apu_tri_lin[4]));
  LED led_17 (.in(apu_tri_lin[5]));
  LED led_18 (.in(apu_tri_lin[6]));
  LED TRI_RELOAD (.in(apu_tri_lin[7]));
  _2A03_APU apu (
    .nRES_PIN(nRES), .RDY__CPU(apu_rdy__cpu), .R_W__CPU(core_r_w), .nIRQ_CPU(apu_nirq_cpu),
    .nNMI_CPU(apu_nnmi_cpu), .nNMI_PIN(1'b1), .R_W__EXT(apu_r_w__ext), .DBG__EXT(1'b0),
    .PHI0__CPU(apu_phi0__cpu), .nIRQ_PIN(1'b1), .Data_to_CPU(apu_data_to_cpu), .Data_from_CPU(wram_db_out),
    .AUX_A(apu_aux_a), .AUX_B(apu_aux_b), .CPU_Ax(core_addr), .AB(apu_ab), .DB_out_EXT(apu_db_out_ext),
    .PHI1_FromCore(core_phi1), .PHI2_FromCore(core_phi2), .CLK(XTAL_out), .RND(apu_rnd), .TRI(apu_tri),
    .SQB(apu_sqb), .SQA(apu_sqa), .DMC(apu_dmc), .SQA_F(apu_sqa_f), .SW_B(apu_sw_b), .SW_A(apu_sw_a),
    .SQB_F(apu_sqb_f), .N_ENV(apu_n_env), .RMODE(apu_rmode), .N_REQ(apu_n_req), .SQB_ENV(apu_sqb_env),
    .SQB_DUTY(apu_sqb_duty), .SQA_DUTY(apu_sqa_duty), .SQA_ENV(apu_sqa_env), .TRI_LIN(apu_tri_lin),
    .TRI_FREQ(apu_tri_freq), .DMCF(apu_dmcf), .DMC_ENIRQ(apu_dmc_enirq), .DMC_LOOP(apu_dmc_loop),
    .SAMPLE_LENGTH(apu_sample_length), .SAMPLE_BUF(apu_sample_buf), .SAMPLE_ADR(apu_sample_adr));  // open: OUT0, OUT1, OUT2, nIN0, nIN1, M2__EXT, DB_in_EXT
  LED led_19 (.in(apu_sqa_f[0]));
  LED led_20 (.in(apu_sqa_f[1]));
  LED led_21 (.in(apu_sqa_f[2]));
  LED led_22 (.in(apu_sqa_f[3]));
  LED led_23 (.in(apu_sqa_f[4]));
  LED led_24 (.in(apu_sqa_f[5]));
  LED led_25 (.in(apu_sqa_f[6]));
  LED led_26 (.in(apu_sqa_f[7]));
  LED led_27 (.in(apu_sqa_f[8]));
  LED led_28 (.in(apu_sqa_f[9]));
  LED led_29 (.in(apu_sqa_f[10]));
  LED SQA_ENV (.in(apu_sqa_env[0]));
  LED led_30 (.in(apu_sqa_env[1]));
  LED led_31 (.in(apu_sqa_env[2]));
  LED led_32 (.in(apu_sqa_env[3]));
  LED ENVDIS (.in(apu_sqa_env[4]));
  LED HALT_SQA (.in(apu_sqa_env[5]));
  LED SQA_DUTY (.in(apu_sqa_duty[0]));
  LED led_33 (.in(apu_sqa_duty[1]));
  LED led_34 (.in(apu_sw_a[0]));
  LED led_35 (.in(apu_sw_a[1]));
  LED led_36 (.in(apu_sw_a[2]));
  LED led_37 (.in(apu_sw_a[3]));
  LED led_38 (.in(apu_sw_a[4]));
  LED led_39 (.in(apu_sw_a[5]));
  LED led_40 (.in(apu_sw_a[6]));
  LED led_41 (.in(apu_sw_a[7]));
  LED led_42 (.in(apu_sqb_f[0]));
  LED led_43 (.in(apu_sqb_f[1]));
  LED led_44 (.in(apu_sqb_f[2]));
  LED led_45 (.in(apu_sqb_f[3]));
  LED led_46 (.in(apu_sqb_f[4]));
  LED led_47 (.in(apu_sqb_f[5]));
  LED led_48 (.in(apu_sqb_f[6]));
  LED led_49 (.in(apu_sqb_f[7]));
  LED led_50 (.in(apu_sqb_f[8]));
  LED led_51 (.in(apu_sqb_f[9]));
  LED led_52 (.in(apu_sqb_f[10]));
  LED SQB_ENV (.in(apu_sqb_env[0]));
  LED led_53 (.in(apu_sqb_env[1]));
  LED led_54 (.in(apu_sqb_env[2]));
  LED led_55 (.in(apu_sqb_env[3]));
  LED ENVDIS_2 (.in(apu_sqb_env[4]));
  LED HALT_SQB (.in(apu_sqb_env[5]));
  WRAM wram (
    .M2(apu_phi0__cpu), .Addr(apu_ab), .DB_in(apu_db_out_ext), .R_W(apu_r_w__ext), .nRES(nRES),
    .DB_out(wram_db_out));
  Fake6502 core (
    .PHI0(apu_phi0__cpu), .RDY(apu_rdy__cpu), .SO(1'b1), .nNMI(apu_nnmi_cpu), .nIRQ(apu_nirq_cpu),
    .nRES(nRES), .DB_in(apu_data_to_cpu), .PHI1(core_phi1), .PHI2(core_phi2), .R_W(core_r_w),
    .Addr(core_addr), .DB_out(wram_db_out), .out_15(core_out_15), .in_8(Next_RegOp_out));  // open: SYNC
  LED SQB_DUTY (.in(apu_sqb_duty[0]));
  LED led_56 (.in(apu_sqb_duty[1]));
  LED led_57 (.in(apu_sw_b[0]));
  LED led_58 (.in(apu_sw_b[1]));
  LED led_59 (.in(apu_sw_b[2]));
  LED led_60 (.in(apu_sw_b[3]));
  LED led_61 (.in(apu_sw_b[4]));
  LED led_62 (.in(apu_sw_b[5]));
  LED led_63 (.in(apu_sw_b[6]));
  LED led_64 (.in(apu_sw_b[7]));
  Button Next_RegOp (.out(Next_RegOp_out));
  // Probe on core_out_15
  LED RMODE (.in(apu_rmode));
  LED NFREQ (.in(apu_n_req[0]));
  LED led_65 (.in(apu_n_req[1]));
  LED led_66 (.in(apu_n_req[2]));
  LED led_67 (.in(apu_n_req[3]));
  LED N_ENV (.in(apu_n_env[0]));
  LED led_68 (.in(apu_n_env[1]));
  LED led_69 (.in(apu_n_env[2]));
  LED led_70 (.in(apu_n_env[3]));
  LED ENVDIS_3 (.in(apu_n_env[4]));
  LED HALT_NOISE (.in(apu_n_env[5]));
  AUXDumper dumper (.PHI1(core_phi1), .AUX({1'b0, apu_aux_b, apu_aux_a}), .Addr(dumper_addr), .Data(dumper_data));
  LED SAMPLE_ADR (.in(apu_sample_adr[0]));
  LED led_71 (.in(apu_sample_adr[1]));
  LED led_72 (.in(apu_sample_adr[2]));
  LED led_73 (.in(apu_sample_adr[3]));
  LED led_74 (.in(apu_sample_adr[4]));
  LED led_75 (.in(apu_sample_adr[5]));
  LED led_76 (.in(apu_sample_adr[6]));
  LED led_77 (.in(apu_sample_adr[7]));
  LED SAMPLE_LEN (.in(apu_sample_length[0]));
  LED led_78 (.in(apu_sample_length[1]));
  LED led_79 (.in(apu_sample_length[2]));
  LED led_80 (.in(apu_sample_length[3]));
  LED led_81 (.in(apu_sample_length[4]));
  LED led_82 (.in(apu_sample_length[5]));
  LED led_83 (.in(apu_sample_length[6]));
  LED led_84 (.in(apu_sample_length[7]));
  Hex_Digit_Display hex_digit_display_1 (.value(transp_latch_q_3));  // open: dp
  Register #(.width(16), .trigger("high")) transp_latch (
    .D(core_addr), .en(core_addr[14]), .Q({transp_latch_q_3, transp_latch_q_2, transp_latch_q}),
    .clk(core_phi2));  // open: clr
  LED SAMPLE_BUF (.in(apu_sample_buf[0]));
  LED led_85 (.in(apu_sample_buf[1]));
  LED led_86 (.in(apu_sample_buf[2]));
  LED led_87 (.in(apu_sample_buf[3]));
  LED led_88 (.in(apu_sample_buf[4]));
  LED led_89 (.in(apu_sample_buf[5]));
  LED led_90 (.in(apu_sample_buf[6]));
  LED led_91 (.in(apu_sample_buf[7]));
  LED DMC_FREQ (.in(apu_dmcf[0]));
  LED led_92 (.in(apu_dmcf[1]));
  LED led_93 (.in(apu_dmcf[2]));
  LED led_94 (.in(apu_dmcf[3]));
  LED LOOP (.in(apu_dmc_loop));
  LED ENIRQ (.in(apu_dmc_enirq));
  Hex_Digit_Display hex_digit_display_2 (.value(transp_latch_q[7:4]));  // open: dp
  Hex_Digit_Display hex_digit_display_3 (.value(transp_latch_q_2));  // open: dp
  Hex_Digit_Display hex_digit_display_4 (.value(transp_latch_q[3:0]));  // open: dp
  RAM #(.addrWidth(24), .dataWidth(32), .bus("asynch")) ram_1 (
    .addr(dumper_addr), .data(dumper_data), .sel(1'b1), .ld(1'b0), .clr(1'b0));
  LED DB (.in(wram_db_out[0]));
  LED led_95 (.in(wram_db_out[1]));
  LED led_96 (.in(wram_db_out[2]));
  LED led_97 (.in(wram_db_out[3]));
  LED led_98 (.in(wram_db_out[4]));
  LED led_99 (.in(wram_db_out[5]));
  LED led_100 (.in(wram_db_out[6]));
  LED led_101 (.in(wram_db_out[7]));

  // Notes on the sheet:
  //   TRI_F
  //   TRI_LIN
  //   SQA_F
  //   SW_A
  //   N.C.
  //   SQB_F
  //   SW_B
  //   Load regdump here
  //   Last APU Register
  //   Taram-param-pam. Pam! Peep, peep, peep. Pipipipip, pip, pibibip
endmodule

module AUXDumper (
  input  PHI1,
  input  [23:0] AUX,
  output [23:0] Addr,
  output [31:0] Data
);

  wire adder_1_p3, and_1_out, counter_1_carry, counter_2_q, counter_3_q, multiplier_1_p3, s_r_ff_1_q;
  wire [31:0] aux_a_1_a, aux_b_1_a;

  AUX_A aux_a_1 (.d(AUX[7:0]), .a(aux_a_1_a));
  AUX_B aux_b_1 (.d(AUX[23:8]), .a(aux_b_1_a));
  and and_1 (and_1_out, PHI1, ~s_r_ff_1_q);  // AND_Gate
  Counter #(.width(23), .max('h7fffff), .ongoal("stay")) counter_1 (
    .Q(Addr[23:1]), .carry(counter_1_carry), .clk(and_1_out));  // open: load, D, count, clr
  // Multiplier multiplier_1: pin names not known; wires that end beside it: aux_a_1_a, 32'h3ecccccd, multiplier_1_p3
  Counter #(.width(1), .max('h1)) counter_2 (.Q(counter_2_q), .clk(and_1_out));  // open: load, D, count, carry, clr
  Counter #(.width(1), .max('h1), .trigger("falling")) counter_3 (
    .Q(counter_3_q), .clk(and_1_out));  // open: load, D, count, carry, clr
  // Adder adder_1: pin names not known; wires that end beside it: multiplier_1_p3, aux_b_1_a, adder_1_p3
  xnor xnor_1 (Addr[0], counter_2_q, counter_3_q);
  // Divider divider_1: pin names not known; wires that end beside it: adder_1_p3, 32'h40000000, Data
  S_R_Flip_Flop s_r_ff_1 (.S(counter_1_carry), .Q(s_r_ff_1_q));  // open: clk, R, Qn, preset, reset, en

  // Notes on the sheet:
  //   * 0.4
  //   float->uint32_t Convert: https://gregstoll.com/~gregstoll/floattohex/
  //   a + b
  //   The invention of the org to make the ADDR tick EVERY half cycle.
  //    : 2
  //   normalized samples in range [0.0f; 1.0f]
endmodule

module AUX_A (
  input  [7:0] d,
  output [31:0] a
);

  ROM #(.dataWidth(32)) rom_1 (.addr(d), .data(a), .sel(1'b1));

  // Notes on the sheet:
  //   0...255
  //   contents of rom_1 (hex, n*v repeats v):
  //   3ab77b8e 3d12a8ec 3d924925 3ddadec7 3e118b0c 3e3577e6 3e59364e 3e7cc69c 3e901495 3ea1af28 3eb33333
  //   3ec4a0e1 3ed5f85c 3ee739ce 3ef86563 3f04bda1 3d12a8ec 3d924925 3ddadec7 3e118b0c 3e3577e6 3e59364e
  //   3e7cc69c 3e901495 3ea1af28 3eb33333 3ec4a0e1 3ed5f85c 3ee739ce 3ef86563 3f04bda1 3f0d3dcb 3d924925
  //   3ddadec7 3e118b0c 3e3577e6 3e59364e 3e7cc69c 3e901495 3ea1af28 3eb33333 3ec4a0e1 3ed5f85c 3ee739ce
  //   3ef86563 3f04bda1 3f0d3dcb 3f15b343 3ddadec7 3e118b0c 3e3577e6 3e59364e 3e7cc69c 3e901495 3ea1af28
  //   3eb33333 3ec4a0e1 3ed5f85c 3ee739ce 3ef86563 3f04bda1 3f0d3dcb 3f15b343 3f1e1e1e 3e118b0c 3e3577e6
  //   3e59364e 3e7cc69c 3e901495 3ea1af28 3eb33333 3ec4a0e1 3ed5f85c 3ee739ce 3ef86563 3f04bda1 3f0d3dcb
  //   3f15b343 3f1e1e1e 3f267e6f 3e3577e6 3e59364e 3e7cc69c 3e901495 3ea1af28 3eb33333 3ec4a0e1 3ed5f85c
  //   3ee739ce 3ef86563 3f04bda1 3f0d3dcb 3f15b343 3f1e1e1e 3f267e6f 3f2ed44b 3e59364e 3e7cc69c 3e901495
  //   3ea1af28 3eb33333 3ec4a0e1 3ed5f85c 3ee739ce 3ef86563 3f04bda1 3f0d3dcb 3f15b343 3f1e1e1e 3f267e6f
  //   3f2ed44b 3f371fc4 3e7cc69c 3e901495 3ea1af28 3eb33333 3ec4a0e1 3ed5f85c 3ee739ce 3ef86563 3f04bda1
  //   3f0d3dcb 3f15b343 3f1e1e1e 3f267e6f 3f2ed44b 3f371fc4 3f3f60ef 3e901495 3ea1af28 3eb33333 3ec4a0e1
  //   3ed5f85c 3ee739ce 3ef86563 3f04bda1 3f0d3dcb 3f15b343 3f1e1e1e 3f267e6f 3f2ed44b 3f371fc4 3f3f60ef
  //   3f4797dd 3ea1af28 3eb33333 3ec4a0e1 3ed5f85c 3ee739ce 3ef86563 3f04bda1 3f0d3dcb 3f15b343 3f1e1e1e
  //   3f267e6f 3f2ed44b 3f371fc4 3f3f60ef 3f4797dd 3f4fc4a3 3eb33333 3ec4a0e1 3ed5f85c 3ee739ce 3ef86563
  //   3f04bda1 3f0d3dcb 3f15b343 3f1e1e1e 3f267e6f 3f2ed44b 3f371fc4 3f3f60ef 3f4797dd 3f4fc4a3 3f57e753
  //   3ec4a0e1 3ed5f85c 3ee739ce 3ef86563 3f04bda1 3f0d3dcb 3f15b343 3f1e1e1e 3f267e6f 3f2ed44b 3f371fc4
  //   3f3f60ef 3f4797dd 3f4fc4a3 3f57e753 3f600000 3ed5f85c 3ee739ce 3ef86563 3f04bda1 3f0d3dcb 3f15b343
  //   3f1e1e1e 3f267e6f 3f2ed44b 3f371fc4 3f3f60ef 3f4797dd 3f4fc4a3 3f57e753 3f600000 3f680ebc 3ee739ce
  //   3ef86563 3f04bda1 3f0d3dcb 3f15b343 3f1e1e1e 3f267e6f 3f2ed44b 3f371fc4 3f3f60ef 3f4797dd 3f4fc4a3
  //   3f57e753 3f600000 3f680ebc 3f701399 3ef86563 3f04bda1 3f0d3dcb 3f15b343 3f1e1e1e 3f267e6f 3f2ed44b
  //   3f371fc4 3f3f60ef 3f4797dd 3f4fc4a3 3f57e753 3f600000 3f680ebc 3f701399 3f780eaa 3f04bda1 3f0d3dcb
  //   3f15b343 3f1e1e1e 3f267e6f 3f2ed44b 3f371fc4 3f3f60ef 3f4797dd 3f4fc4a3 3f57e753 3f600000 3f680ebc
  //   3f701399 3f780eaa 3f800000
endmodule

module AUX_B (
  input  [15:0] d,
  output [31:0] a
);

  ROM #(.addrWidth(15), .dataWidth(32)) rom_1 (.addr(d[14:0]), .data(a), .sel(1'b1));

  // Notes on the sheet:
  //   0...32767
  //   contents of rom_1 (hex, n*v repeats v):
  //   39f0dbd4 3cc007b4 3d3f0e2a 3d8e915b 3dbd229a 3deb3ca3 3e0c709f 3e230913 3e39688b 3e4f8fdb 3e657fd7
  //   3e7b394d 3e885e84 3e9305e6 3e9d932f 3ea806be 3c40856f 3d0fa7f6 3d6e36ed 3da5e8fe 3dd43e69 3e010ec1
  //   3e17c406 3e2e3fe1 3e44832b 3e5a8eb7 3e706356 3e8300eb 3e8db57e 3e984fc8 3ea2d028 3ead36fd 3cc007b4
  //   3d3f0e2a 3d8e915b 3dbd229a 3deb3ca3 3e0c709f 3e230913 3e39688b 3e4f8fdb 3e657fd7 3e7b394d 3e885e84
  //   3e9305e6 3e9d932f 3ea806be 3eb260f0 3d0fa7f6 3d6e36ed 3da5e8fe 3dd43e69 3e010ec1 3e17c406 3e2e3fe1
  //   3e44832b 3e5a8eb7 3e706356 3e8300eb 3e8db57e 3e984fc8 3ea2d028 3ead36fd 3eb784a4 3d3f0e2a 3d8e915b
  //   3dbd229a 3deb3ca3 3e0c709f 3e230913 3e39688b 3e4f8fdb 3e657fd7 3e7b394d 3e885e84 3e9305e6 3e9d932f
  //   3ea806be 3eb260f0 3ebca222 3d6e36ed 3da5e8fe 3dd43e69 3e010ec1 3e17c406 3e2e3fe1 3e44832b 3e5a8eb7
  //   3e706356 3e8300eb 3e8db57e 3e984fc8 3ea2d028 3ead36fd 3eb784a4 3ec1b977 3d8e915b 3dbd229a 3deb3ca3
  //   3e0c709f 3e230913 3e39688b 3e4f8fdb 3e657fd7 3e7b394d 3e885e84 3e9305e6 3e9d932f 3ea806be 3eb260f0
  //   3ebca222 3ec6caae 3da5e8fe 3dd43e69 3e010ec1 3e17c406 3e2e3fe1 3e44832b 3e5a8eb7 3e706356 3e8300eb
  //   3e8db57e 3e984fc8 3ea2d028 3ead36fd 3eb784a4 3ec1b977 3ecbd5d1 3dbd229a 3deb3ca3 3e0c709f 3e230913
  //   3e39688b 3e4f8fdb 3e657fd7 3e7b394d 3e885e84 3e9305e6 3e9d932f 3ea806be 3eb260f0 3ebca222 3ec6caae
  //   3ed0daec 3dd43e69 3e010ec1 3e17c406 3e2e3fe1 3e44832b 3e5a8eb7 3e706356 3e8300eb 3e8db57e 3e984fc8
  //   3ea2d028 3ead36fd 3eb784a4 3ec1b977 3ecbd5d1 3ed5da09 3deb3ca3 3e0c709f 3e230913 3e39688b 3e4f8fdb
  //   3e657fd7 3e7b394d 3e885e84 3e9305e6 3e9d932f 3ea806be 3eb260f0 3ebca222 3ec6caae 3ed0daec 3edad333
  //   3e010ec1 3e17c406 3e2e3fe1 3e44832b 3e5a8eb7 3e706356 3e8300eb 3e8db57e 3e984fc8 3ea2d028 3ead36fd
  //   3eb784a4 3ec1b977 3ecbd5d1 3ed5da09 3edfc674 3e0c709f 3e230913 3e39688b 3e4f8fdb 3e657fd7 3e7b394d
  //   3e885e84 3e9305e6 3e9d932f 3ea806be 3eb260f0 3ebca222 3ec6caae 3ed0daec 3edad333 3ee4b3d8 3e17c406
  //   3e2e3fe1 3e44832b 3e5a8eb7 3e706356 3e8300eb 3e8db57e 3e984fc8 3ea2d028 3ead36fd 3eb784a4 3ec1b977
  //   3ecbd5d1 3ed5da09 3edfc674 3ee99b68 3e230913 3e39688b 3e4f8fdb 3e657fd7 3e7b394d 3e885e84 3e9305e6
  //   3e9d932f 3ea806be 3eb260f0 3ebca222 3ec6caae 3ed0daec 3edad333 3ee4b3d8 3eee7d2e 3e2e3fe1 3e44832b
  //   3e5a8eb7 3e706356 3e8300eb 3e8db57e 3e984fc8 3ea2d028 3ead36fd 3eb784a4 3ec1b977 3ecbd5d1 3ed5da09
  //   3edfc674 3ee99b68 3ef35936 3bc0c48a 3cefbb5a 3d56aa32 3d9a40f1 3dc8b438 3df6b0bb 3e121c1f 3e28a641
  //   3e3ef79a 3e551102 3e6af34a 3e804f9f 3e8b0ad4 3e95aba7 3ea03278 3eaa9fa7 3c9034de 3d2762c6 3d82da35
  //   3db1898a 3ddfc135 3e06c180 3e1d6856 3e33d5f9 3e4a0b3f 3e6008fd 3e75d001 3e85b08c 3e905e84 3e9af24a
  //   3ea56c3e 3eafccbf 3cefbb5a 3d56aa32 3d9a40f1 3dc8b438 3df6b0bb 3e121c1f 3e28a641 3e3ef79a 3e551102
  //   3e6af34a 3e804f9f 3e8b0ad4 3e95aba7 3ea03278 3eaa9fa7 3eb4f391 3d2762c6 3d82da35 3db1898a 3ddfc135
  //   3e06c180 3e1d6856 3e33d5f9 3e4a0b3f 3e6008fd 3e75d001 3e85b08c 3e905e84 3e9af24a 3ea56c3e 3eafccbf
  //   3eba1429 3d56aa32 3d9a40f1 3dc8b438 3df6b0bb 3e121c1f 3e28a641 3e3ef79a 3e551102 3e6af34a 3e804f9f
  //   3e8b0ad4 3e95aba7 3ea03278 3eaa9fa7 3eb4f391 3ebf2e91 3d82da35 3db1898a 3ddfc135 3e06c180 3e1d6856
  //   3e33d5f9 3e4a0b3f 3e6008fd 3e75d001 3e85b08c 3e905e84 3e9af24a 3ea56c3e 3eafccbf 3eba1429 3ec442d6
  //   3d9a40f1 3dc8b438 3df6b0bb 3e121c1f 3e28a641 3e3ef79a 3e551102 3e6af34a 3e804f9f 3e8b0ad4 3e95aba7
  //   3ea03278 3eaa9fa7 3eb4f391 3ebf2e91 3ec95101 3db1898a 3ddfc135 3e06c180 3e1d6856 3e33d5f9 3e4a0b3f
  //   3e6008fd 3e75d001 3e85b08c 3e905e84 3e9af24a 3ea56c3e 3eafccbf 3eba1429 3ec442d6 3ece591f 3dc8b438
  //   3df6b0bb 3e121c1f 3e28a641 3e3ef79a 3e551102 3e6af34a 3e804f9f 3e8b0ad4 3e95aba7 3ea03278 3eaa9fa7
  //   3eb4f391 3ebf2e91 3ec95101 3ed35b39 3ddfc135 3e06c180 3e1d6856 3e33d5f9 3e4a0b3f 3e6008fd 3e75d001
  //   3e85b08c 3e905e84 3e9af24a 3ea56c3e 3eafccbf 3eba1429 3ec442d6 3ece591f 3ed8575b 3df6b0bb 3e121c1f
  //   3e28a641 3e3ef79a 3e551102 3e6af34a 3e804f9f 3e8b0ad4 3e95aba7 3ea03278 3eaa9fa7 3eb4f391 3ebf2e91
  //   3ec95101 3ed35b39 3edd4d90 3e06c180 3e1d6856 3e33d5f9 3e4a0b3f 3e6008fd 3e75d001 3e85b08c 3e905e84
  //   3e9af24a 3ea56c3e 3eafccbf 3eba1429 3ec4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
endmodule

module Fake6502 (
  input  PHI0,
  input  RDY,
  input  SO,
  input  nNMI,
  input  nIRQ,
  input  nRES,
  input  [7:0] DB_in,
  input  in_8,
  output PHI1,
  output PHI2,
  output R_W,
  output SYNC,
  output [15:0] Addr,
  output [7:0] DB_out,
  output [31:0] out_15
);

  wire [23:0] redump_redump_addr;
  wire [31:0] rom_1_data;

  ROM #(.addrWidth(24), .dataWidth(32)) rom_1 (.addr(redump_redump_addr), .data(rom_1_data), .sel(1'b1));
  RegDumpProcessor redump (
    .PHI0(PHI0), .regdump_data(rom_1_data), .Core_R_W(R_W), .Core_AB(Addr), .Core_DB(DB_out),
    .redump_addr(redump_redump_addr), .out_8(out_15), .in_2(in_8));
  not not_1 (PHI1, PHI0);

  assign PHI2 = PHI0;
  assign SYNC = 1'b0;

  // Notes on the sheet:
  //   N.C.
  //   N.C.
  //   N.C.
  //   Load regdump here
  //   contents of rom_1 (hex, n*v repeats v):
  //   2 10 6 1f15 9 c017 98 1f15 6 10 a0d 1000 4 1004 4 100c 6 8 6 f15 2 214 2f1 116 6 16 1b3 116 6 16 210
  //   1000 4 1004 4 100c 6 8 6 f15 100 1000 c 1004 c 8 c 100c 2 214 4f6 116 6 16 1b3 116 6 16 297 1000 c
  //   1004 c 8 c 100c 2 214 4f6 116 6 16 1b3 116 6 16 297 1000 c 1004 c 8 c 100c 2 214 4f5 116 6 16 1b3
  //   116 6 16 297 1000 c 1004 c 8 c 100c 2 214 4f6 116 6 16 1b3 116 6 16 297 1000 c 1004 c 8 c 100c 2 214
  //   4f6 116 6 16 1b3 116 6 16 297 1000 c 1004 c 8 c 100c 2 214 2f0 116 6 16 1b3 116 6 16 297 1000 c 1004
  //   c 8 c 100c 2 1000 4 1004 4 100c 6 8 6 f15 100 1000 c 1004 c 8 c 100c 2 1000 4 1004 4 100c 6 8 6 f15
  //   4c1 800c 8 80d 15 80f 8 2 174 ff08 8 809 15 80b 8 c90a 101 1004 8 805 15 807 8 6 101 1000 8 801 ec
  //   8d10 b 1011 b 4012 b a913 b f15 7 f15 6a1e 214 2f0 116 6 16 1b3 116 6 16 359 800c 8 80d 15 80f 8 e
  //   132 ff08 8 809 15 80b 8 d50a af 1004 8 805 b7 1000 8 801 695b 214 4f6 116 6 16 1b3 116 6 16 2f9 800c
  //   8 80d 13a ff08 8 809 15 80b 8 c90a af 1004 8 805 b7 1000 8 801 67ca 214 4f5 116 6 16 1b3 116 6 16
  //   359 800c 8 80d 15 80f 8 790e 163 ff08 8 809 15 80b 8 c90a af 1004 8 805 b7 1000 8 801 6725 214 4f6
  //   116 6 16 1b3 116 6 16 359 800c 8 80d 15 80f 8 e 132 ff08 8 809 15 80b 8 d50a af 1004 8 805 b7 1000 8
  //   801 6756 214 4f6 116 6 16 1b3 116 6 16 2f9 800c 8 80d 13a ff08 8 809 15 80b 8 c90a af 1004 8 805 b7
  //   1000 8 801 67c7 214 4f6 116 6 16 1b3 116 6 16 2f9 800c 8 80d 13a ff08 8 809 15 80b 8 be0a af 1004 8
  //   805 b7 1000 8 801 67ca 214 4f5 116 6 16 1b3 116 6 16 359 800c 8 80d 15 80f 8 790e 1ca ff08 8 809 15
  //   80b 8 c90a af 1004 8 805 b7 1000 8 801 66bd 214 4f5 116 6 16 1b3 116 6 16 359 800c 8 80d 15 80f 8 e
  //   132 ff08 8 809 15 80b 8 d50a af 1004 8 805 b7 1000 8 801 6758 214 4f6 116 6 16 1b3 116 6 16 328 800c
  //   8 80d 13a ff08 8 809 15 80b 8 c90a af 1004 8 805 b7 1000 8 801 6797 214 4f5 116 6 16 1b3 116 6 16
  //   359 800c 8 80d 15 80f 8 790e 179 ff08 8 809 15 80b 8 c90a af 1004 8 805 b7 1000 8 801 6711 214 4f6
  //   116 6 16 1b3 116 6 16 359 800c 8 80d 15 80f 8 e 132 ff08 8 809 15 80b 8 d50a af 1004 8 805 b7 1000 8
  //   801 6752 214 4f6 116 6 16 1b3 116 6 16 340 800c 8 80d 13a ff08 8 809 15 80b 8 e20a af 1004 8 805 b7
  //   1000 8 801 6785 214 4f5 116 6 16 1b3 116 6 16 2f9 800c 8 80d 13a ff08 8 809 15 80b 8 f00a af 1004 8
  //   805 b7 1000 8 801 67c9 214 4f6 116 6 16 1b3 116 6 16 2f9 800c 8 80d 10a 8 8 809 b7 1004 8 805 b7
  //   1000 8 801 680f 214 4f5 116 6 16 1b3 116 6 16 359 800c 8 80d 15 80f 8 790e 1c3 ff08 8 809 15 80b 8
  //   c90a af 1004 8 805 b7 1000 8 801 66c5 214 4f6 116 6 16 1b3 116 6 16 359 800c 8 80d 15 80f 8 e 132
  //   ff08 8 809 15 80b 8 d50a af 1004 8 805 b7 1000 8 801 6754 214 4f6 116 6 16 1b3 116 6 16 33f 800c 8
  //   80d 13a ff08 8 809 15 80b 8 e20a af 1004 8 805 b7 1000 8 801 6783 214 4f6 116 6 16 1b3 116 6 16 2f9
  //   800c 8 80d 13a ff08 8 809 15 80b 8 f00a af 1004 8 805 b7 1000 8 801 67cb 214 4f6 116 6 16 1b3 116 6
  //   16 2f9 800c 8 80d 10a 8 8 809 b7 1004 8 805 b7 1000 8 801 680d 214 4f5 116 6 16 1b3 116 6 16 359
  //   800c 8 80d 15 80f 8 790e 179 ff08 8 809 15 90b 8 400a af 1004 8 805 b7 1000 8 801 670e 214 4f5 116 6
  //   16 1b3 116 6 16 359 800c 8 80d 15 80f 8 e 132 ff08 8 809 15 90b 8 530a af 1004 8 805 b7 1000 8 801
  //   6756 214 4f6 116 6 16 1b3 116 6 16 33f 800c 8 80d 13a ff08 8 809 15 90b 8 670a af 1004 8 805 b7 1000
  //   8 801 6786 214 4f5 116 6 16 1b3 116 6 16 2f9 800c 8 80d 13a ff08 8 809 15 90b 8 7d0a af 1004 8 805
  //   b7 1000 8 801 67c8 214 4f5 116 6 16 1b3 116 6 16 2f9 800c 8 80d 10a 8 8 809 b7 1004 8 805 b7 1000 8
  //   801 6810 214 4f6 116 6 16 1b3 116 6 16 359 800c 8 80d 15 80f 8 790e 1c3 ff08 8 809 15 90b 8 400a af
  //   1004 8 805 b7 1000 8 801 66c3 214 4f6 116 6 16 1b3 116 6 16 359 800c 8 80d 15 80f 8 e 132 ff08 8 809
  //   15 90b 8 530a af 1004 8 805 b7 1000 8 801 6756 214 4f6 116 6 16 1b3 116 6 16 33f 800c 8 80d 13a ff08
  //   8 809 15 90b 8 670a af 1004 8 805 b7 1000 8 801 6783 214 4f6 116 6 16 1b3 116 6 16 2f9 800c 8 80d
  //   13a ff08 8 809 15 90b 8 7d0a af 1004 8 805 b7 1000 8 801 67c8 214 4f5 116 6 16 1b3 116 6 16 2f9 800c
  //   8 80d 10a 8 8 809 b7 1004 8 805 b7 1000 8 801 6810 214 4f6 116 6 16 1b3 116 6 16 359 800c 8 80d 15
  //   80f 8 790e 1a8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
endmodule

module WRAM (
  input  M2,
  input  [15:0] Addr,
  input  [7:0] DB_in,
  input  R_W,
  input  nRES,
  output [7:0] DB_out
);

  wire and_1_out, comparator_1_eq, comparator_1_gt, nor_1_out, or_1_out;
  wire [7:0] ram_1_data;

  nor nor_1 (nor_1_out, Addr[11], Addr[12], Addr[13], Addr[14], Addr[15]);
  Comparator #(.width(16)) comparator_1 (
    .a(16'h8000), .b(Addr), .gt(comparator_1_gt), .eq(comparator_1_eq));  // open: lt
  and and_1 (and_1_out, nor_1_out, or_1_out);
  or or_1 (or_1_out, comparator_1_gt, comparator_1_eq);
  // NOT_Gate not_1 is placed but not wired
  RAM #(.addrWidth(16), .bus("separate")) ram_1 (
    .addr(Addr), .din(DB_in), .data(ram_1_data), .sel(1'b1), .ld(R_W));  // open: str, clk, clr
  Register #(.trigger("high")) register_1 (.D(ram_1_data), .Q(DB_out), .clk(1'b1));  // open: en, clr

  // Notes on the sheet:
  //   Load 64K CPU Memory dump here (with DPCM samples)
endmodule

module RegDumpProcessor (
  input  PHI0,
  input  in_2,
  input  [31:0] regdump_data,
  output Core_R_W,
  output [15:0] Core_AB,
  output [7:0] Core_DB,
  output [23:0] redump_addr,
  output [31:0] out_8
);

  wire and_1_out, and_2_out, cnt_ovf_reg_q, comparator_1_eq, comparator_1_gt, comparator_2_eq,
       comparator_3_gt, multiplexer_1_out, multiplexer_2_out, not_1_out, or_1_out, or_2_out, or_3_out;
  wire [7:0] regop_word_q_2, undriven;
  wire [15:0] or_4_out;
  wire [31:0] delta_phi_word_q, multiplexer_3_out, multiplexer_4_out, regop_word_q, subtractor_1_out;

  or or_1 (or_1_out, in_2, cnt_ovf_reg_q);
  Multiplexer #(.enable("false")) multiplexer_1 (.in0(1'b1), .in1(1'b1), .out(multiplexer_1_out), .sel(or_1_out));
  Multiplexer #(.enable("false")) multiplexer_2 (.in0(1'b1), .in1(1'b0), .out(multiplexer_2_out), .sel(or_1_out));
  Multiplexer #(.width(32), .enable("false")) multiplexer_3 (
    .in0(regdump_data), .in1(32'h20), .out(multiplexer_3_out), .sel(in_2));
  Register #(.width(32)) delta_phi_word (.D(regdump_data), .Q(delta_phi_word_q), .clk(cnt_ovf_reg_q));  // open: en, clr
  or or_2 (or_2_out, comparator_1_gt, comparator_1_eq);
  Comparator #(.width(32)) comparator_1 (
    .a(regdump_data), .b(32'h2), .gt(comparator_1_gt), .eq(comparator_1_eq));  // open: lt
  Subtractor #(.width(32)) subtractor_1 (.a(regdump_data), .b(32'h2), .out(subtractor_1_out));  // open: bin, bout
  Counter #(.width(32), .max('hffffffff), .ongoal("stay")) phi_dec_cnt (
    .load(multiplexer_1_out), .D(multiplexer_3_out), .count(multiplexer_2_out), .Q(out_8), .clk(PHI0));  // open: carry, clr
  Multiplexer #(.width(32), .enable("false")) multiplexer_4 (
    .in0(32'h1), .in1(subtractor_1_out), .out(multiplexer_4_out), .sel(or_2_out));
  Register #(.width(32)) regop_word (
    .D(regdump_data), .Q({regop_word_q[31:16], regop_word_q_2, regop_word_q[7:0]}), .clk(and_1_out),
    .clr(cnt_ovf_reg_q));  // open: en
  Comparator #(.width(32)) comparator_2 (.a(out_8), .b({32{1'b0}}), .eq(comparator_2_eq));  // open: gt, lt
  Comparator #(.width(32)) comparator_3 (.a(delta_phi_word_q), .b({32{1'b0}}), .gt(comparator_3_gt));  // open: eq, lt
  Register #(.width(1)) cnt_ovf_reg (.D(comparator_2_eq), .Q(cnt_ovf_reg_q), .clk(PHI0));  // open: en, clr
  and and_1 (and_1_out, PHI0, comparator_3_gt, comparator_2_eq, ~cnt_ovf_reg_q);  // AND_Gate
  or or_3 (or_3_out, and_1_out, cnt_ovf_reg_q);
  assign or_4_out = 16'h4000 | {{11{1'b0}}, regop_word_q[4:0]};  // OR_Gate or_4, 16 bits wide
  not not_1 (not_1_out, regop_word_q[7]);
  Multiplexer #(.enable("false")) multiplexer_5 (.in0(1'b1), .in1(regop_word_q[7]), .out(Core_R_W), .sel(and_1_out));
  Multiplexer #(.width(16), .enable("false")) multiplexer_6 (
    .in0({16{1'b0}}), .in1(or_4_out), .out(Core_AB), .sel(and_1_out));
  Multiplexer #(.width(8), .enable("false")) multiplexer_7 (
    .in0(undriven), .in1(regop_word_q_2), .out(Core_DB), .sel(and_2_out));
  and and_2 (and_2_out, and_1_out, not_1_out);
  Counter #(.width(24), .max('hffffff), .ongoal("stay"), .trigger("falling")) addr_cnt (
    .load(1'b0), .count(1'b1), .Q(redump_addr), .clk(or_3_out));  // open: D, carry, clr

  // Notes on the sheet:
  //   https://github.com/emu-russia/breaknes/blob/main/BreaksAPU/NSFPlayerInterop/RegDumpProcessor.cpp
  //   Load/Decrement Setup (1: Load; 0: Decrement)
  //   Do RegOp
  //   Load PHI Counter
  //   RegOp Setup
  //   Reg Index (0-0x1f)
  //   Reg Address
  //   Value (if write)
  //   1: Read register
  //   Default: Read address 0x0000
  //   1: RegOp + Write
  //   Falling edge
endmodule
