// Logisim project 6502_Evo.circ as structural Verilog: 62 circuits, main circuit BogusSystem
module BogusSystem (
  input  RDY,
  input  SO,
  input  n_NMI,
  input  n_IRQ,
  input  n_RES
);

  wire mos6502_phi1, mos6502_phi2, mos6502_rnw, mos6502_sync, not_1_out, not_2_out, PHI0_out;
  wire [7:0] mem_dout, mos6502_d_out0;
  wire [15:0] mos6502_a0;

  Clock PHI0 (.out(PHI0_out));
  MOS_6502 mos6502 (
    .n_RES(n_RES), .SO(SO), .PHI0(PHI0_out), .D0(mem_dout[0]), .D1(mem_dout[1]), .D2(mem_dout[2]),
    .D3(mem_dout[3]), .D4(mem_dout[4]), .D5(mem_dout[5]), .D6(mem_dout[6]), .D7(mem_dout[7]), .n_NMI(n_NMI),
    .n_IRQ(n_IRQ), .RDY(RDY), .PHI2(mos6502_phi2), .RnW(mos6502_rnw), .D_out0(mos6502_d_out0[0]),
    .D_out1(mos6502_d_out0[1]), .D_out2(mos6502_d_out0[2]), .D_out3(mos6502_d_out0[3]),
    .D_out4(mos6502_d_out0[4]), .D_out5(mos6502_d_out0[5]), .D_out6(mos6502_d_out0[6]),
    .D_out7(mos6502_d_out0[7]), .A8(mos6502_a0[8]), .A9(mos6502_a0[9]), .A10(mos6502_a0[10]),
    .A11(mos6502_a0[11]), .A12(mos6502_a0[12]), .A13(mos6502_a0[13]), .A14(mos6502_a0[14]),
    .A0(mos6502_a0[0]), .A1(mos6502_a0[1]), .A2(mos6502_a0[2]), .A3(mos6502_a0[3]), .A4(mos6502_a0[4]),
    .A5(mos6502_a0[5]), .A6(mos6502_a0[6]), .A7(mos6502_a0[7]), .SYNC(mos6502_sync), .A15(mos6502_a0[15]),
    .PHI1(mos6502_phi1));
  // NoConnect on mos6502_phi1
  not not_1 (not_1_out, mos6502_rnw);
  Counter #(.max('hffffffff), .width(32)) counter_1 (
    .count(1'b1), .clk(mos6502_phi2), .clr(not_2_out));  // open: load, D, Q, carry, up
  not not_2 (not_2_out, n_RES);
  RAM #(.addrWidth(16)) mem (
    .addr(mos6502_a0), .we(not_1_out), .oe(mos6502_rnw), .clk(mos6502_phi2), .din(mos6502_d_out0),
    .dout(mem_dout));
  Counter #(.max('hffffffff), .width(32)) counter_2 (
    .count(1'b1), .clk(mos6502_sync), .clr(not_2_out));  // open: load, D, Q, carry, up

  // Notes on the sheet:
  //   CLK Counter
  //   Instr Counter
endmodule

module MOS_6502 (
  input  n_NMI,
  input  n_IRQ,
  input  RDY,
  input  n_RES,
  input  SO,
  input  PHI0,
  input  D0,
  input  D1,
  input  D2,
  input  D3,
  input  D4,
  input  D5,
  input  D6,
  input  D7,
  output PHI1,
  output PHI2,
  output RnW,
  output SYNC,
  output A0,
  output A1,
  output A2,
  output A3,
  output A4,
  output A5,
  output A6,
  output A7,
  output D_out0,
  output D_out1,
  output D_out2,
  output D_out3,
  output D_out4,
  output D_out5,
  output A8,
  output A9,
  output A10,
  output A11,
  output A12,
  output A13,
  output A14,
  output A15,
  output D_out6,
  output D_out7
);

  wire bot_acr, bot_avr, decoder_trans_1_x0, decoder_trans_1_x1, decoder_trans_1_x2, decoder_trans_1_x3,
       decoder_trans_1_x4, decoder_trans_1_x5, decoder_trans_1_x6, decoder_trans_1_x7, decoder_trans_1_x8,
       decoder_trans_1_x9, decoder_trans_1_x10, decoder_trans_1_x11, decoder_trans_1_x12,
       decoder_trans_1_x13, decoder_trans_1_x14, decoder_trans_1_x15, decoder_trans_1_x16,
       decoder_trans_1_x17, decoder_trans_1_x18, decoder_trans_1_x19, decoder_trans_1_x20,
       decoder_trans_1_x21, decoder_trans_1_x22, decoder_trans_1_x23, decoder_trans_1_x24,
       decoder_trans_1_x25, decoder_trans_1_x26, decoder_trans_1_x27, decoder_trans_1_x28,
       decoder_trans_1_x29, decoder_trans_1_x30, decoder_trans_1_x31, decoder_trans_1_x32,
       decoder_trans_1_x33, decoder_trans_1_x34, decoder_trans_1_x35, decoder_trans_1_x36,
       decoder_trans_1_x37, decoder_trans_1_x38, decoder_trans_1_x39, decoder_trans_1_x40,
       decoder_trans_1_x41, decoder_trans_1_x42, decoder_trans_1_x43, decoder_trans_1_x44,
       decoder_trans_1_x45, decoder_trans_1_x46, decoder_trans_1_x47, decoder_trans_1_x48,
       decoder_trans_1_x49, decoder_trans_1_x50, decoder_trans_1_x51, decoder_trans_1_x52,
       decoder_trans_1_x53, decoder_trans_1_x54, decoder_trans_1_x55, decoder_trans_1_x56,
       decoder_trans_1_x57, decoder_trans_1_x58, decoder_trans_1_x59, decoder_trans_1_x60,
       decoder_trans_1_x61, decoder_trans_1_x62, decoder_trans_1_x63, decoder_trans_1_x64,
       decoder_trans_1_x65, decoder_trans_1_x66, decoder_trans_1_x67, decoder_trans_1_x68,
       decoder_trans_1_x69, decoder_trans_1_x70, decoder_trans_1_x71, decoder_trans_1_x72,
       decoder_trans_1_x73, decoder_trans_1_x74, decoder_trans_1_x75, decoder_trans_1_x76,
       decoder_trans_1_x77, decoder_trans_1_x78, decoder_trans_1_x79, decoder_trans_1_x80,
       decoder_trans_1_x81, decoder_trans_1_x82, decoder_trans_1_x83, decoder_trans_1_x84,
       decoder_trans_1_x85, decoder_trans_1_x86, decoder_trans_1_x87, decoder_trans_1_x88,
       decoder_trans_1_x89, decoder_trans_1_x90, decoder_trans_1_x91, decoder_trans_1_x92,
       decoder_trans_1_x93, decoder_trans_1_x94, decoder_trans_1_x95, decoder_trans_1_x96,
       decoder_trans_1_x97, decoder_trans_1_x98, decoder_trans_1_x99, decoder_trans_1_x100,
       decoder_trans_1_x101, decoder_trans_1_x102, decoder_trans_1_x103, decoder_trans_1_x104,
       decoder_trans_1_x105, decoder_trans_1_x106, decoder_trans_1_x107, decoder_trans_1_x108,
       decoder_trans_1_x109, decoder_trans_1_x110, decoder_trans_1_x111, decoder_trans_1_x112,
       decoder_trans_1_x113, decoder_trans_1_x114, decoder_trans_1_x115, decoder_trans_1_x116,
       decoder_trans_1_x117, decoder_trans_1_x118, decoder_trans_1_x119, decoder_trans_1_x120,
       decoder_trans_1_x121, decoder_trans_1_x122, decoder_trans_1_x123, decoder_trans_1_x124,
       decoder_trans_1_x125, decoder_trans_1_x126, decoder_trans_1_x127, decoder_trans_1_x128,
       decoder_trans_1_x129, IR_ir0, IR_ir1, IR_ir2, IR_ir3, IR_ir4, IR_ir5, IR_ir6, IR_ir7, irqp_ff_q,
       irqp_latch_not_q, nmip_ff_q, not_1_out, not_2_out, not_3_out, not_4_out, not_5_out, not_6_out,
       prdy_latch1_not_q, prdy_latch2_not_q, predecode_1_n_implied, predecode_1_n_pd0, predecode_1_n_pd1,
       predecode_1_n_pd2, predecode_1_n_pd3, predecode_1_n_pd4, predecode_1_n_pd5, predecode_1_n_pd6,
       predecode_1_n_pd7, predecode_1_n_twocycle, random_logic_1_acr_c, random_logic_1_db_c,
       random_logic_1_db_n, random_logic_1_db_p, random_logic_1_db_v, random_logic_1_dbz_z,
       random_logic_1_fetch, random_logic_1_ir5_c, random_logic_1_ir5_d, random_logic_1_ir5_i,
       random_logic_1_n_acin, random_logic_1_n_c_out, random_logic_1_n_d_out, random_logic_1_n_daa,
       random_logic_1_n_dsa, random_logic_1_n_i_out, random_logic_1_n_ipc, random_logic_1_n_n_out,
       random_logic_1_n_t0, random_logic_1_n_t1x, random_logic_1_n_t2, random_logic_1_n_t3,
       random_logic_1_n_t4, random_logic_1_n_t5, random_logic_1_n_v_out, random_logic_1_n_z_out,
       random_logic_1_p_db, random_logic_1_t1, random_logic_1_wr, random_logic_1_z_ir, random_logic_1_z_v,
       resp_ff_nq, resp_latch_not_q;
  wire [7:0] bot_db_out, random_logic_1_db_out0;
  wire [43:0] random_logic_1_y_sb;

  buf buffer_1 (SYNC, random_logic_1_t1);
  not not_1 (not_1_out, n_NMI);
  DECODER_TRANS decoder_trans_1 (
    .IR6(IR_ir6), .IR5(IR_ir5), .n_T0(random_logic_1_n_t0), .n_T1X(random_logic_1_n_t1x),
    .n_T5(random_logic_1_n_t5), .n_T4(random_logic_1_n_t4), .n_T3(random_logic_1_n_t3),
    .n_T2(random_logic_1_n_t2), .IR0(IR_ir0), .IR1(IR_ir1), .IR7(IR_ir7), .IR4(IR_ir4), .IR3(IR_ir3),
    .IR2(IR_ir2), .x10(decoder_trans_1_x10), .x11(decoder_trans_1_x11), .x12(decoder_trans_1_x12),
    .x13(decoder_trans_1_x13), .x14(decoder_trans_1_x14), .x15(decoder_trans_1_x15),
    .x16(decoder_trans_1_x16), .x17(decoder_trans_1_x17), .x18(decoder_trans_1_x18),
    .x19(decoder_trans_1_x19), .x20(decoder_trans_1_x20), .x21(decoder_trans_1_x21),
    .x22(decoder_trans_1_x22), .x23(decoder_trans_1_x23), .x24(decoder_trans_1_x24),
    .x25(decoder_trans_1_x25), .x26(decoder_trans_1_x26), .x27(decoder_trans_1_x27),
    .x28(decoder_trans_1_x28), .x29(decoder_trans_1_x29), .x30(decoder_trans_1_x30),
    .x31(decoder_trans_1_x31), .x32(decoder_trans_1_x32), .x33(decoder_trans_1_x33),
    .x34(decoder_trans_1_x34), .x35(decoder_trans_1_x35), .x36(decoder_trans_1_x36),
    .x37(decoder_trans_1_x37), .x38(decoder_trans_1_x38), .x39(decoder_trans_1_x39),
    .x40(decoder_trans_1_x40), .x41(decoder_trans_1_x41), .x42(decoder_trans_1_x42),
    .x43(decoder_trans_1_x43), .x44(decoder_trans_1_x44), .x0(decoder_trans_1_x0), .x45(decoder_trans_1_x45),
    .x46(decoder_trans_1_x46), .x47(decoder_trans_1_x47), .x48(decoder_trans_1_x48),
    .x49(decoder_trans_1_x49), .x50(decoder_trans_1_x50), .x51(decoder_trans_1_x51),
    .x52(decoder_trans_1_x52), .x53(decoder_trans_1_x53), .x1(decoder_trans_1_x1), .x54(decoder_trans_1_x54),
    .x55(decoder_trans_1_x55), .x56(decoder_trans_1_x56), .x57(decoder_trans_1_x57),
    .x58(decoder_trans_1_x58), .x59(decoder_trans_1_x59), .x60(decoder_trans_1_x60),
    .x61(decoder_trans_1_x61), .x62(decoder_trans_1_x62), .x2(decoder_trans_1_x2), .x63(decoder_trans_1_x63),
    .x64(decoder_trans_1_x64), .x65(decoder_trans_1_x65), .x66(decoder_trans_1_x66),
    .x67(decoder_trans_1_x67), .x68(decoder_trans_1_x68), .x69(decoder_trans_1_x69),
    .x70(decoder_trans_1_x70), .x71(decoder_trans_1_x71), .x72(decoder_trans_1_x72), .x3(decoder_trans_1_x3),
    .x73(decoder_trans_1_x73), .x74(decoder_trans_1_x74), .x75(decoder_trans_1_x75),
    .x76(decoder_trans_1_x76), .x77(decoder_trans_1_x77), .x78(decoder_trans_1_x78),
    .x79(decoder_trans_1_x79), .x80(decoder_trans_1_x80), .x81(decoder_trans_1_x81), .x4(decoder_trans_1_x4),
    .x82(decoder_trans_1_x82), .x83(decoder_trans_1_x83), .x84(decoder_trans_1_x84),
    .x85(decoder_trans_1_x85), .x86(decoder_trans_1_x86), .x87(decoder_trans_1_x87),
    .x88(decoder_trans_1_x88), .x89(decoder_trans_1_x89), .x90(decoder_trans_1_x90), .x5(decoder_trans_1_x5),
    .x91(decoder_trans_1_x91), .x92(decoder_trans_1_x92), .x93(decoder_trans_1_x93),
    .x94(decoder_trans_1_x94), .x95(decoder_trans_1_x95), .x96(decoder_trans_1_x96),
    .x97(decoder_trans_1_x97), .x98(decoder_trans_1_x98), .x99(decoder_trans_1_x99),
    .x100(decoder_trans_1_x100), .x101(decoder_trans_1_x101), .x102(decoder_trans_1_x102),
    .x103(decoder_trans_1_x103), .x104(decoder_trans_1_x104), .x105(decoder_trans_1_x105),
    .x106(decoder_trans_1_x106), .x107(decoder_trans_1_x107), .x108(decoder_trans_1_x108),
    .x109(decoder_trans_1_x109), .x6(decoder_trans_1_x6), .x110(decoder_trans_1_x110),
    .x111(decoder_trans_1_x111), .x112(decoder_trans_1_x112), .x113(decoder_trans_1_x113),
    .x114(decoder_trans_1_x114), .x115(decoder_trans_1_x115), .x116(decoder_trans_1_x116),
    .x117(decoder_trans_1_x117), .x118(decoder_trans_1_x118), .x119(decoder_trans_1_x119),
    .x7(decoder_trans_1_x7), .x120(decoder_trans_1_x120), .x121(decoder_trans_1_x121),
    .x122(decoder_trans_1_x122), .x123(decoder_trans_1_x123), .x124(decoder_trans_1_x124),
    .x125(decoder_trans_1_x125), .x126(decoder_trans_1_x126), .x127(decoder_trans_1_x127),
    .x128(decoder_trans_1_x128), .x129(decoder_trans_1_x129), .x8(decoder_trans_1_x8), .x9(decoder_trans_1_x9));
  RANDOM_LOGIC random_logic_1 (
    .X26(decoder_trans_1_x26), .X27(decoder_trans_1_x27), .X28(decoder_trans_1_x28),
    .X29(decoder_trans_1_x29), .n_NMIP(not_2_out), .RESP(resp_latch_not_q), .n_IRQP(irqp_latch_not_q),
    .AVR(bot_avr), .ACR(bot_acr), .SO(SO), .X30(decoder_trans_1_x30), .X31(decoder_trans_1_x31),
    .X32(decoder_trans_1_x32), .X33(decoder_trans_1_x33), .X34(decoder_trans_1_x34),
    .X35(decoder_trans_1_x35), .X36(decoder_trans_1_x36), .X37(decoder_trans_1_x37),
    .X38(decoder_trans_1_x38), .X39(decoder_trans_1_x39), .X40(decoder_trans_1_x40),
    .X41(decoder_trans_1_x41), .X42(decoder_trans_1_x42), .X43(decoder_trans_1_x43), .X0(decoder_trans_1_x0),
    .X44(decoder_trans_1_x44), .X45(decoder_trans_1_x45), .X46(decoder_trans_1_x46),
    .X47(decoder_trans_1_x47), .X48(decoder_trans_1_x48), .X49(decoder_trans_1_x49),
    .X50(decoder_trans_1_x50), .X51(decoder_trans_1_x51), .X52(decoder_trans_1_x52), .X1(decoder_trans_1_x1),
    .X53(decoder_trans_1_x53), .X54(decoder_trans_1_x54), .X55(decoder_trans_1_x55),
    .X56(decoder_trans_1_x56), .X57(decoder_trans_1_x57), .X58(decoder_trans_1_x58),
    .X59(decoder_trans_1_x59), .X60(decoder_trans_1_x60), .X61(decoder_trans_1_x61), .X2(decoder_trans_1_x2),
    .X62(decoder_trans_1_x62), .X63(decoder_trans_1_x63), .X64(decoder_trans_1_x64),
    .X65(decoder_trans_1_x65), .X66(decoder_trans_1_x66), .X67(decoder_trans_1_x67),
    .X68(decoder_trans_1_x68), .X69(decoder_trans_1_x69), .X70(decoder_trans_1_x70), .X3(decoder_trans_1_x3),
    .X71(decoder_trans_1_x71), .X72(decoder_trans_1_x72), .X73(decoder_trans_1_x73),
    .X74(decoder_trans_1_x74), .X75(decoder_trans_1_x75), .X76(decoder_trans_1_x76),
    .X77(decoder_trans_1_x77), .X78(decoder_trans_1_x78), .X79(decoder_trans_1_x79), .X4(decoder_trans_1_x4),
    .X80(decoder_trans_1_x80), .X81(decoder_trans_1_x81), .X82(decoder_trans_1_x82),
    .X83(decoder_trans_1_x83), .X84(decoder_trans_1_x84), .X85(decoder_trans_1_x85),
    .X86(decoder_trans_1_x86), .X87(decoder_trans_1_x87), .X88(decoder_trans_1_x88),
    .X89(decoder_trans_1_x89), .X5(decoder_trans_1_x5), .X90(decoder_trans_1_x90), .X91(decoder_trans_1_x91),
    .X92(decoder_trans_1_x92), .X93(decoder_trans_1_x93), .X94(decoder_trans_1_x94),
    .X95(decoder_trans_1_x95), .X96(decoder_trans_1_x96), .X97(decoder_trans_1_x97),
    .X98(decoder_trans_1_x98), .X6(decoder_trans_1_x6), .X99(decoder_trans_1_x99),
    .X100(decoder_trans_1_x100), .X101(decoder_trans_1_x101), .X102(decoder_trans_1_x102),
    .X103(decoder_trans_1_x103), .X104(decoder_trans_1_x104), .X105(decoder_trans_1_x105),
    .X106(decoder_trans_1_x106), .X107(decoder_trans_1_x107), .X7(decoder_trans_1_x7),
    .X108(decoder_trans_1_x108), .X109(decoder_trans_1_x109), .X110(decoder_trans_1_x110),
    .X111(decoder_trans_1_x111), .X112(decoder_trans_1_x112), .X113(decoder_trans_1_x113),
    .X114(decoder_trans_1_x114), .X115(decoder_trans_1_x115), .X116(decoder_trans_1_x116),
    .X8(decoder_trans_1_x8), .X117(decoder_trans_1_x117), .X118(decoder_trans_1_x118),
    .X119(decoder_trans_1_x119), .X120(decoder_trans_1_x120), .X121(decoder_trans_1_x121),
    .X122(decoder_trans_1_x122), .X123(decoder_trans_1_x123), .X124(decoder_trans_1_x124),
    .X125(decoder_trans_1_x125), .X9(decoder_trans_1_x9), .X126(decoder_trans_1_x126),
    .X127(decoder_trans_1_x127), .X128(decoder_trans_1_x128), .X129(decoder_trans_1_x129),
    .DB7(bot_db_out[7]), .DB6(bot_db_out[6]), .DB5(bot_db_out[5]), .DB4(bot_db_out[4]), .DB3(bot_db_out[3]),
    .DB2(bot_db_out[2]), .PHI2(PHI2), .IR0(IR_ir0), .n_IR5(not_6_out), .n_TWOCYCLE(predecode_1_n_twocycle),
    .n_IMPLIED(predecode_1_n_implied), .RDY(RDY), .n_PRDY(prdy_latch2_not_q), .PHI1(PHI1),
    .DB1(bot_db_out[1]), .DB0(bot_db_out[0]), .X10(decoder_trans_1_x10), .X11(decoder_trans_1_x11),
    .X12(decoder_trans_1_x12), .X13(decoder_trans_1_x13), .X14(decoder_trans_1_x14),
    .X15(decoder_trans_1_x15), .X16(decoder_trans_1_x16), .X17(decoder_trans_1_x17),
    .X18(decoder_trans_1_x18), .X19(decoder_trans_1_x19), .X20(decoder_trans_1_x20),
    .X21(decoder_trans_1_x21), .X22(decoder_trans_1_x22), .X23(decoder_trans_1_x23),
    .X24(decoder_trans_1_x24), .X25(decoder_trans_1_x25), .n_C_OUT(random_logic_1_n_c_out),
    .n_N_OUT(random_logic_1_n_n_out), .n_Z_OUT(random_logic_1_n_z_out), .NDB_ADD(random_logic_1_y_sb[8]),
    .DB_ADD(random_logic_1_y_sb[9]), .Z_ADD(random_logic_1_y_sb[10]), .SB_ADD(random_logic_1_y_sb[11]),
    .ADL_ADD(random_logic_1_y_sb[12]), .ANDS(random_logic_1_y_sb[13]), .EORS(random_logic_1_y_sb[14]),
    .ORS(random_logic_1_y_sb[15]), .n_ACIN(random_logic_1_n_acin), .SUMS(random_logic_1_y_sb[17]),
    .n_DAA(random_logic_1_n_daa), .ADD_SB7(random_logic_1_y_sb[18]), .ADD_SB06(random_logic_1_y_sb[19]),
    .ADD_ADL(random_logic_1_y_sb[20]), .n_DSA(random_logic_1_n_dsa), .SRS(random_logic_1_y_sb[16]),
    .DL_ADL(random_logic_1_y_sb[41]), .DL_DB(random_logic_1_y_sb[43]), .DL_ADH(random_logic_1_y_sb[42]),
    .ADH_ABH(random_logic_1_y_sb[32]), .ADL_ABL(random_logic_1_y_sb[33]), .SB_AC(random_logic_1_y_sb[21]),
    .AC_SB(random_logic_1_y_sb[22]), .Z_ADH0(random_logic_1_y_sb[37]), .Z_ADH17(random_logic_1_y_sb[38]),
    .Z_ADL0(random_logic_1_y_sb[34]), .AC_DB(random_logic_1_y_sb[23]), .SB_DB(random_logic_1_y_sb[39]),
    .SB_ADH(random_logic_1_y_sb[40]), .ADL_PCL(random_logic_1_y_sb[28]), .PCL_PCL(random_logic_1_y_sb[29]),
    .PCH_ADH(random_logic_1_y_sb[26]), .PCL_ADL(random_logic_1_y_sb[30]), .PCH_DB(random_logic_1_y_sb[27]),
    .PCL_DB(random_logic_1_y_sb[31]), .Z_ADL1(random_logic_1_y_sb[35]), .ADH_PCH(random_logic_1_y_sb[24]),
    .PCH_PCH(random_logic_1_y_sb[25]), .Z_IR(random_logic_1_z_ir), .T1(random_logic_1_t1),
    .n_T1X(random_logic_1_n_t1x), .Z_ADL2(random_logic_1_y_sb[36]), .n_IPC(random_logic_1_n_ipc),
    .P_DB(random_logic_1_p_db), .IR5_I(random_logic_1_ir5_i), .IR5_C(random_logic_1_ir5_c),
    .IR5_D(random_logic_1_ir5_d), .Z_V(random_logic_1_z_v), .DB_out7(random_logic_1_db_out0[7]),
    .ACR_C(random_logic_1_acr_c), .DB_out6(random_logic_1_db_out0[6]), .DBZ_Z(random_logic_1_dbz_z),
    .DB_out5(random_logic_1_db_out0[5]), .DB_N(random_logic_1_db_n), .Y_SB(random_logic_1_y_sb[0]),
    .DB_out4(random_logic_1_db_out0[4]), .DB_P(random_logic_1_db_p), .DB_out3(random_logic_1_db_out0[3]),
    .DB_C(random_logic_1_db_c), .DB_out2(random_logic_1_db_out0[2]), .DB_V(random_logic_1_db_v),
    .DB_out1(random_logic_1_db_out0[1]), .DB_out0(random_logic_1_db_out0[0]), .n_T2(random_logic_1_n_t2),
    .n_T3(random_logic_1_n_t3), .n_T4(random_logic_1_n_t4), .n_T5(random_logic_1_n_t5),
    .WR(random_logic_1_wr), .FETCH(random_logic_1_fetch), .n_T0(random_logic_1_n_t0),
    .X_SB(random_logic_1_y_sb[2]), .SB_Y(random_logic_1_y_sb[1]), .SB_X(random_logic_1_y_sb[3]),
    .S_SB(random_logic_1_y_sb[5]), .S_ADL(random_logic_1_y_sb[4]), .SB_S(random_logic_1_y_sb[6]),
    .S_S(random_logic_1_y_sb[7]), .n_V_OUT(random_logic_1_n_v_out), .n_I_OUT(random_logic_1_n_i_out),
    .n_D_OUT(random_logic_1_n_d_out));
  INT_FF nmip_ff (.phi2(PHI2), .d(not_1_out), .q(nmip_ff_q));  // open: nq
  not not_2 (not_2_out, nmip_ff_q);
  not not_3 (not_3_out, n_IRQ);
  INT_FF irqp_ff (.phi2(PHI2), .d(not_3_out), .q(irqp_ff_q));  // open: nq
  D_Latch irqp_latch (.EN(PHI1), .D(irqp_ff_q), .NOT_Q(irqp_latch_not_q));  // open: Q
  not not_4 (not_4_out, RDY);
  D_Latch prdy_latch1 (.EN(PHI2), .D(not_4_out), .NOT_Q(prdy_latch1_not_q));  // open: Q
  BotPart bot (
    .PHI1(PHI1), .PHI2(PHI2), .WR(random_logic_1_wr), .bop(random_logic_1_y_sb),
    .n_ACIN(random_logic_1_n_acin), .n_DAA(random_logic_1_n_daa), .n_DSA(random_logic_1_n_dsa),
    .n_IPC(random_logic_1_n_ipc), .DB_in(random_logic_1_db_out0),
    .DataBus_in({D7, D6, D5, D4, D3, D2, D1, D0}),
    .A({A15, A14, A13, A12, A11, A10, A9, A8, A7, A6, A5, A4, A3, A2, A1, A0}), .DB_out(bot_db_out),
    .DataBus_out({D_out7, D_out6, D_out5, D_out4, D_out3, D_out2, D_out1, D_out0}), .ACR(bot_acr),
    .AVR(bot_avr));
  not not_5 (not_5_out, n_RES);
  D_Latch prdy_latch2 (.EN(PHI1), .D(prdy_latch1_not_q), .NOT_Q(prdy_latch2_not_q));  // open: Q
  INT_FF resp_ff (.phi2(PHI2), .d(not_5_out), .nq(resp_ff_nq));  // open: q
  D_Latch resp_latch (.EN(PHI1), .D(resp_ff_nq), .NOT_Q(resp_latch_not_q));  // open: Q
  CLOCKGEN clockgen_1 (.PHI0(PHI0), .PHI2(PHI2), .PHI1(PHI1));
  not not_6 (not_6_out, IR_ir5);
  D_Latch rw_latch (.EN(PHI1), .D(random_logic_1_wr), .NOT_Q(RnW));  // open: Q
  IR_Logic IR (
    .n_in0(predecode_1_n_pd0), .n_in1(predecode_1_n_pd1), .n_in2(predecode_1_n_pd2),
    .n_in3(predecode_1_n_pd3), .n_in4(predecode_1_n_pd4), .n_in5(predecode_1_n_pd5),
    .n_in6(predecode_1_n_pd6), .n_in7(predecode_1_n_pd7), .FETCH(random_logic_1_fetch), .PHI1(PHI1),
    .IR0(IR_ir0), .IR1(IR_ir1), .IR2(IR_ir2), .IR3(IR_ir3), .IR4(IR_ir4), .IR5(IR_ir5), .IR6(IR_ir6),
    .IR7(IR_ir7));
  PREDECODE predecode_1 (
    .D0(D0), .PHI2(PHI2), .D1(D1), .D2(D2), .D3(D3), .D4(D4), .D5(D5), .Z_IR(random_logic_1_z_ir), .D6(D6),
    .D7(D7), .n_PD0(predecode_1_n_pd0), .n_PD1(predecode_1_n_pd1), .n_PD2(predecode_1_n_pd2),
    .n_PD3(predecode_1_n_pd3), .n_PD4(predecode_1_n_pd4), .n_PD5(predecode_1_n_pd5),
    .n_PD6(predecode_1_n_pd6), .n_PD7(predecode_1_n_pd7), .n_TWOCYCLE(predecode_1_n_twocycle),
    .n_IMPLIED(predecode_1_n_implied));

  // Notes on the sheet:
  //   PHI2
  //   PHI1
  //   PHI2
  //   T1
  //   PHI1
  //   /NMIP
  //   /IRQP
  //   /PRDY
  //   The pin layout corresponds to the real chip
  //   nQ !!!
  //   RESP
  //   PHI2
  //   PHI1
  //   WR
  //   PHI1
  //   PHI2
endmodule

module CLOCKGEN (
  input  PHI0,
  output PHI2,
  output PHI1
);

  wire not_1_out;

  not not_1 (not_1_out, PHI0);
  not not_2 (PHI1, PHI0);
  not not_3 (PHI2, not_1_out);
endmodule

module IR_Logic (
  input  FETCH,
  input  PHI1,
  input  n_in0,
  input  n_in1,
  input  n_in2,
  input  n_in3,
  input  n_in4,
  input  n_in5,
  input  n_in6,
  input  n_in7,
  output IR0,
  output IR1,
  output IR2,
  output IR3,
  output IR4,
  output IR5,
  output IR6,
  output IR7
);

  wire and_1_out;

  and and_1 (and_1_out, FETCH, PHI1);
  D_Latch d_latch_1 (.EN(and_1_out), .D(n_in0), .NOT_Q(IR0));  // open: Q
  D_Latch d_latch_2 (.EN(and_1_out), .D(n_in1), .NOT_Q(IR1));  // open: Q
  D_Latch d_latch_3 (.EN(and_1_out), .D(n_in2), .NOT_Q(IR2));  // open: Q
  D_Latch d_latch_4 (.EN(and_1_out), .D(n_in3), .NOT_Q(IR3));  // open: Q
  D_Latch d_latch_5 (.EN(and_1_out), .D(n_in4), .NOT_Q(IR4));  // open: Q
  D_Latch d_latch_6 (.EN(and_1_out), .D(n_in5), .NOT_Q(IR5));  // open: Q
  D_Latch d_latch_7 (.EN(and_1_out), .D(n_in6), .NOT_Q(IR6));  // open: Q
  D_Latch d_latch_8 (.EN(and_1_out), .D(n_in7), .NOT_Q(IR7));  // open: Q
endmodule

// DECODER
module DECODER_TRANS (
  input  n_T5,
  input  n_T4,
  input  n_T3,
  input  n_T2,
  input  IR0,
  input  IR1,
  input  IR7,
  input  IR4,
  input  IR3,
  input  IR2,
  input  IR6,
  input  IR5,
  input  n_T0,
  input  n_T1X,
  output x0,
  output x1,
  output x2,
  output x3,
  output x4,
  output x5,
  output x6,
  output x7,
  output x8,
  output x9,
  output x10,
  output x11,
  output x12,
  output x13,
  output x14,
  output x15,
  output x16,
  output x17,
  output x18,
  output x19,
  output x20,
  output x21,
  output x22,
  output x23,
  output x24,
  output x25,
  output x26,
  output x27,
  output x28,
  output x29,
  output x30,
  output x31,
  output x32,
  output x33,
  output x34,
  output x35,
  output x36,
  output x37,
  output x38,
  output x39,
  output x40,
  output x41,
  output x42,
  output x43,
  output x44,
  output x45,
  output x46,
  output x47,
  output x48,
  output x49,
  output x50,
  output x51,
  output x52,
  output x53,
  output x54,
  output x55,
  output x56,
  output x57,
  output x58,
  output x59,
  output x60,
  output x61,
  output x62,
  output x63,
  output x64,
  output x65,
  output x66,
  output x67,
  output x68,
  output x69,
  output x70,
  output x71,
  output x72,
  output x73,
  output x74,
  output x75,
  output x76,
  output x77,
  output x78,
  output x79,
  output x80,
  output x81,
  output x82,
  output x83,
  output x84,
  output x85,
  output x86,
  output x87,
  output x88,
  output x89,
  output x90,
  output x91,
  output x92,
  output x93,
  output x94,
  output x95,
  output x96,
  output x97,
  output x98,
  output x99,
  output x100,
  output x101,
  output x102,
  output x103,
  output x104,
  output x105,
  output x106,
  output x107,
  output x108,
  output x109,
  output x110,
  output x111,
  output x112,
  output x113,
  output x114,
  output x115,
  output x116,
  output x117,
  output x118,
  output x119,
  output x120,
  output x121,
  output x122,
  output x123,
  output x124,
  output x125,
  output x126,
  output x127,
  output x128,
  output x129
);

  wire not_1_out, not_2_out, not_3_out, not_4_out, not_5_out, not_6_out, not_7_out, not_8_out, or_1_out;

  not not_1 (not_1_out, IR1);
  or or_1 (or_1_out, IR0, IR1);
  not not_2 (not_2_out, IR0);
  not not_3 (not_3_out, IR7);
  not not_4 (not_4_out, IR4);
  not not_5 (not_5_out, IR3);
  not not_6 (not_6_out, IR2);
  not not_7 (not_7_out, IR6);
  not not_8 (not_8_out, IR5);
  Pull_Resistor #(.pull(1)) pull_resistor_1 (.node(x0));
  Pull_Resistor #(.pull(1)) pull_resistor_2 (.node(x1));
  Transistor #(.\type ("n")) transistor_1 (.in(1'b0), .out(x1), .gate(n_T3));
  Transistor #(.\type ("n")) transistor_2 (.in(1'b0), .out(x0), .gate(or_1_out));
  Transistor #(.\type ("n")) transistor_3 (.in(1'b0), .out(x1), .gate(not_2_out));
  Transistor #(.\type ("n")) transistor_4 (.in(1'b0), .out(x0), .gate(not_3_out));
  Transistor #(.\type ("n")) transistor_5 (.in(1'b0), .out(x1), .gate(not_4_out));
  Transistor #(.\type ("n")) transistor_6 (.in(1'b0), .out(x1), .gate(IR3));
  Transistor #(.\type ("n")) transistor_7 (.in(1'b0), .out(x1), .gate(IR2));
  Transistor #(.\type ("n")) transistor_8 (.in(1'b0), .out(x0), .gate(not_6_out));
  Transistor #(.\type ("n")) transistor_9 (.in(1'b0), .out(x0), .gate(IR6));
  Transistor #(.\type ("n")) transistor_10 (.in(1'b0), .out(x0), .gate(IR5));
  Pull_Resistor #(.pull(1)) pull_resistor_3 (.node(x2));
  Transistor #(.\type ("n")) transistor_11 (.in(1'b0), .out(x2), .gate(n_T2));
  Transistor #(.\type ("n")) transistor_12 (.in(1'b0), .out(x2), .gate(not_2_out));
  Transistor #(.\type ("n")) transistor_13 (.in(1'b0), .out(x2), .gate(not_4_out));
  Transistor #(.\type ("n")) transistor_14 (.in(1'b0), .out(x2), .gate(not_5_out));
  Transistor #(.\type ("n")) transistor_15 (.in(1'b0), .out(x2), .gate(IR2));
  Pull_Resistor #(.pull(1)) pull_resistor_4 (.node(x3));
  Transistor #(.\type ("n")) transistor_16 (.in(1'b0), .out(x3), .gate(or_1_out));
  Transistor #(.\type ("n")) transistor_17 (.in(1'b0), .out(x3), .gate(not_3_out));
  Transistor #(.\type ("n")) transistor_18 (.in(1'b0), .out(x3), .gate(IR4));
  Transistor #(.\type ("n")) transistor_19 (.in(1'b0), .out(x3), .gate(not_5_out));
  Transistor #(.\type ("n")) transistor_20 (.in(1'b0), .out(x3), .gate(IR2));
  Transistor #(.\type ("n")) transistor_21 (.in(1'b0), .out(x3), .gate(IR5));
  Transistor #(.\type ("n")) transistor_22 (.in(1'b0), .out(x3), .gate(n_T0));
  Pull_Resistor #(.pull(1)) pull_resistor_5 (.node(x4));
  Pull_Resistor #(.pull(1)) pull_resistor_6 (.node(x5));
  Transistor #(.\type ("n")) transistor_23 (.in(1'b0), .out(x4), .gate(or_1_out));
  Transistor #(.\type ("n")) transistor_24 (.in(1'b0), .out(x5), .gate(or_1_out));
  Transistor #(.\type ("n")) transistor_25 (.in(1'b0), .out(x4), .gate(not_3_out));
  Transistor #(.\type ("n")) transistor_26 (.in(1'b0), .out(x5), .gate(not_3_out));
  Transistor #(.\type ("n")) transistor_27 (.in(1'b0), .out(x5), .gate(IR4));
  Transistor #(.\type ("n")) transistor_28 (.in(1'b0), .out(x4), .gate(not_4_out));
  Transistor #(.\type ("n")) transistor_29 (.in(1'b0), .out(x4), .gate(not_5_out));
  Transistor #(.\type ("n")) transistor_30 (.in(1'b0), .out(x4), .gate(IR2));
  Transistor #(.\type ("n")) transistor_31 (.in(1'b0), .out(x4), .gate(IR6));
  Transistor #(.\type ("n")) transistor_32 (.in(1'b0), .out(x5), .gate(not_7_out));
  Transistor #(.\type ("n")) transistor_33 (.in(1'b0), .out(x4), .gate(IR5));
  Transistor #(.\type ("n")) transistor_34 (.in(1'b0), .out(x5), .gate(IR5));
  Transistor #(.\type ("n")) transistor_35 (.in(1'b0), .out(x4), .gate(n_T0));
  Transistor #(.\type ("n")) transistor_36 (.in(1'b0), .out(x5), .gate(n_T0));
  Pull_Resistor #(.pull(1)) pull_resistor_7 (.node(x6));
  Transistor #(.\type ("n")) transistor_37 (.in(1'b0), .out(x6), .gate(n_T2));
  Transistor #(.\type ("n")) transistor_38 (.in(1'b0), .out(x6), .gate(not_4_out));
  Transistor #(.\type ("n")) transistor_39 (.in(1'b0), .out(x6), .gate(not_6_out));
  Pull_Resistor #(.pull(1)) pull_resistor_8 (.node(x7));
  Transistor #(.\type ("n")) transistor_40 (.in(1'b0), .out(x7), .gate(not_1_out));
  Transistor #(.\type ("n")) transistor_41 (.in(1'b0), .out(x7), .gate(not_3_out));
  Transistor #(.\type ("n")) transistor_42 (.in(1'b0), .out(x7), .gate(IR6));
  Pull_Resistor #(.pull(1)) pull_resistor_9 (.node(x8));
  Pull_Resistor #(.pull(1)) pull_resistor_10 (.node(x9));
  Transistor #(.\type ("n")) transistor_43 (.in(1'b0), .out(x8), .gate(n_T2));
  Transistor #(.\type ("n")) transistor_44 (.in(1'b0), .out(x9), .gate(not_1_out));
  Transistor #(.\type ("n")) transistor_45 (.in(1'b0), .out(x8), .gate(not_2_out));
  Transistor #(.\type ("n")) transistor_46 (.in(1'b0), .out(x9), .gate(not_3_out));
  Transistor #(.\type ("n")) transistor_47 (.in(1'b0), .out(x8), .gate(IR4));
  Transistor #(.\type ("n")) transistor_48 (.in(1'b0), .out(x9), .gate(IR4));
  Transistor #(.\type ("n")) transistor_49 (.in(1'b0), .out(x8), .gate(IR3));
  Transistor #(.\type ("n")) transistor_50 (.in(1'b0), .out(x9), .gate(not_5_out));
  Transistor #(.\type ("n")) transistor_51 (.in(1'b0), .out(x8), .gate(IR2));
  Transistor #(.\type ("n")) transistor_52 (.in(1'b0), .out(x9), .gate(IR2));
  Transistor #(.\type ("n")) transistor_53 (.in(1'b0), .out(x9), .gate(IR6));
  Transistor #(.\type ("n")) transistor_54 (.in(1'b0), .out(x9), .gate(IR5));
  Transistor #(.\type ("n")) transistor_55 (.in(1'b0), .out(x9), .gate(n_T0));
  Pull_Resistor #(.pull(1)) pull_resistor_11 (.node(x10));
  Transistor #(.\type ("n")) transistor_56 (.in(1'b0), .out(x10), .gate(not_1_out));
  Transistor #(.\type ("n")) transistor_57 (.in(1'b0), .out(x10), .gate(not_3_out));
  Transistor #(.\type ("n")) transistor_58 (.in(1'b0), .out(x10), .gate(IR4));
  Transistor #(.\type ("n")) transistor_59 (.in(1'b0), .out(x10), .gate(not_5_out));
  Transistor #(.\type ("n")) transistor_60 (.in(1'b0), .out(x10), .gate(IR2));
  Transistor #(.\type ("n")) transistor_61 (.in(1'b0), .out(x10), .gate(not_7_out));
  Transistor #(.\type ("n")) transistor_62 (.in(1'b0), .out(x10), .gate(IR5));
  Transistor #(.\type ("n")) transistor_63 (.in(1'b0), .out(x10), .gate(n_T0));
  Pull_Resistor #(.pull(1)) pull_resistor_12 (.node(x11));
  Transistor #(.\type ("n")) transistor_64 (.in(1'b0), .out(x11), .gate(or_1_out));
  Transistor #(.\type ("n")) transistor_65 (.in(1'b0), .out(x11), .gate(not_3_out));
  Transistor #(.\type ("n")) transistor_66 (.in(1'b0), .out(x11), .gate(IR4));
  Transistor #(.\type ("n")) transistor_67 (.in(1'b0), .out(x11), .gate(not_7_out));
  Transistor #(.\type ("n")) transistor_68 (.in(1'b0), .out(x11), .gate(not_8_out));
  Transistor #(.\type ("n")) transistor_69 (.in(1'b0), .out(x11), .gate(n_T0));
  Pull_Resistor #(.pull(1)) pull_resistor_13 (.node(x12));
  Pull_Resistor #(.pull(1)) pull_resistor_14 (.node(x13));
  Transistor #(.\type ("n")) transistor_70 (.in(1'b0), .out(x12), .gate(not_1_out));
  Transistor #(.\type ("n")) transistor_71 (.in(1'b0), .out(x13), .gate(not_1_out));
  Transistor #(.\type ("n")) transistor_72 (.in(1'b0), .out(x12), .gate(not_3_out));
  Transistor #(.\type ("n")) transistor_73 (.in(1'b0), .out(x13), .gate(not_3_out));
  Transistor #(.\type ("n")) transistor_74 (.in(1'b0), .out(x13), .gate(not_4_out));
  Transistor #(.\type ("n")) transistor_75 (.in(1'b0), .out(x13), .gate(not_5_out));
  Transistor #(.\type ("n")) transistor_76 (.in(1'b0), .out(x13), .gate(IR2));
  Transistor #(.\type ("n")) transistor_77 (.in(1'b0), .out(x12), .gate(IR6));
  Transistor #(.\type ("n")) transistor_78 (.in(1'b0), .out(x13), .gate(IR6));
  Transistor #(.\type ("n")) transistor_79 (.in(1'b0), .out(x12), .gate(IR5));
  Transistor #(.\type ("n")) transistor_80 (.in(1'b0), .out(x13), .gate(IR5));
  Transistor #(.\type ("n")) transistor_81 (.in(1'b0), .out(x13), .gate(n_T0));
  Pull_Resistor #(.pull(1)) pull_resistor_15 (.node(x14));
  Transistor #(.\type ("n")) transistor_82 (.in(1'b0), .out(x14), .gate(not_1_out));
  Transistor #(.\type ("n")) transistor_83 (.in(1'b0), .out(x14), .gate(not_3_out));
  Transistor #(.\type ("n")) transistor_84 (.in(1'b0), .out(x14), .gate(IR6));
  Transistor #(.\type ("n")) transistor_85 (.in(1'b0), .out(x14), .gate(not_8_out));
  Transistor #(.\type ("n")) transistor_86 (.in(1'b0), .out(x14), .gate(n_T0));
  Pull_Resistor #(.pull(1)) pull_resistor_16 (.node(x15));
  Transistor #(.\type ("n")) transistor_87 (.in(1'b0), .out(x15), .gate(not_1_out));
  Transistor #(.\type ("n")) transistor_88 (.in(1'b0), .out(x15), .gate(not_3_out));
  Transistor #(.\type ("n")) transistor_89 (.in(1'b0), .out(x15), .gate(IR4));
  Transistor #(.\type ("n")) transistor_90 (.in(1'b0), .out(x15), .gate(not_5_out));
  Transistor #(.\type ("n")) transistor_91 (.in(1'b0), .out(x15), .gate(IR2));
  Transistor #(.\type ("n")) transistor_92 (.in(1'b0), .out(x15), .gate(not_7_out));
  Transistor #(.\type ("n")) transistor_93 (.in(1'b0), .out(x15), .gate(IR5));
  Transistor #(.\type ("n")) transistor_94 (.in(1'b0), .out(x15), .gate(n_T1X));
  Pull_Resistor #(.pull(1)) pull_resistor_17 (.node(x16));
  Pull_Resistor #(.pull(1)) pull_resistor_18 (.node(x17));
  Transistor #(.\type ("n")) transistor_95 (.in(1'b0), .out(x17), .gate(not_1_out));
  Transistor #(.\type ("n")) transistor_96 (.in(1'b0), .out(x16), .gate(or_1_out));
  Transistor #(.\type ("n")) transistor_97 (.in(1'b0), .out(x16), .gate(not_3_out));
  Transistor #(.\type ("n")) transistor_98 (.in(1'b0), .out(x17), .gate(not_3_out));
  Transistor #(.\type ("n")) transistor_99 (.in(1'b0), .out(x16), .gate(IR4));
  Transistor #(.\type ("n")) transistor_100 (.in(1'b0), .out(x17), .gate(not_4_out));
  Transistor #(.\type ("n")) transistor_101 (.in(1'b0), .out(x16), .gate(not_5_out));
  Transistor #(.\type ("n")) transistor_102 (.in(1'b0), .out(x17), .gate(not_5_out));
  Transistor #(.\type ("n")) transistor_103 (.in(1'b0), .out(x16), .gate(IR2));
  Transistor #(.\type ("n")) transistor_104 (.in(1'b0), .out(x17), .gate(IR2));
  Transistor #(.\type ("n")) transistor_105 (.in(1'b0), .out(x17), .gate(IR6));
  Transistor #(.\type ("n")) transistor_106 (.in(1'b0), .out(x16), .gate(not_7_out));
  Transistor #(.\type ("n")) transistor_107 (.in(1'b0), .out(x16), .gate(not_8_out));
  Transistor #(.\type ("n")) transistor_108 (.in(1'b0), .out(x17), .gate(not_8_out));
  Transistor #(.\type ("n")) transistor_109 (.in(1'b0), .out(x17), .gate(n_T0));
  Transistor #(.\type ("n")) transistor_110 (.in(1'b0), .out(x16), .gate(n_T1X));
  Pull_Resistor #(.pull(1)) pull_resistor_19 (.node(x18));
  Transistor #(.\type ("n")) transistor_111 (.in(1'b0), .out(x18), .gate(or_1_out));
  Transistor #(.\type ("n")) transistor_112 (.in(1'b0), .out(x18), .gate(not_3_out));
  Transistor #(.\type ("n")) transistor_113 (.in(1'b0), .out(x18), .gate(IR4));
  Transistor #(.\type ("n")) transistor_114 (.in(1'b0), .out(x18), .gate(not_5_out));
  Transistor #(.\type ("n")) transistor_115 (.in(1'b0), .out(x18), .gate(IR2));
  Transistor #(.\type ("n")) transistor_116 (.in(1'b0), .out(x18), .gate(IR5));
  Transistor #(.\type ("n")) transistor_117 (.in(1'b0), .out(x18), .gate(n_T1X));
  Pull_Resistor #(.pull(1)) pull_resistor_20 (.node(x19));
  Transistor #(.\type ("n")) transistor_118 (.in(1'b0), .out(x19), .gate(or_1_out));
  Transistor #(.\type ("n")) transistor_119 (.in(1'b0), .out(x19), .gate(not_3_out));
  Transistor #(.\type ("n")) transistor_120 (.in(1'b0), .out(x19), .gate(not_6_out));
  Transistor #(.\type ("n")) transistor_121 (.in(1'b0), .out(x19), .gate(IR6));
  Transistor #(.\type ("n")) transistor_122 (.in(1'b0), .out(x19), .gate(not_8_out));
  Transistor #(.\type ("n")) transistor_123 (.in(1'b0), .out(x19), .gate(n_T0));
  Pull_Resistor #(.pull(1)) pull_resistor_21 (.node(x20));
  Transistor #(.\type ("n")) transistor_124 (.in(1'b0), .out(x20), .gate(or_1_out));
  Transistor #(.\type ("n")) transistor_125 (.in(1'b0), .out(x20), .gate(not_3_out));
  Transistor #(.\type ("n")) transistor_126 (.in(1'b0), .out(x20), .gate(IR4));
  Transistor #(.\type ("n")) transistor_127 (.in(1'b0), .out(x20), .gate(IR6));
  Transistor #(.\type ("n")) transistor_128 (.in(1'b0), .out(x20), .gate(not_8_out));
  Transistor #(.\type ("n")) transistor_129 (.in(1'b0), .out(x20), .gate(n_T0));
  Pull_Resistor #(.pull(1)) pull_resistor_22 (.node(x21));
  Transistor #(.\type ("n")) transistor_130 (.in(1'b0), .out(x21), .gate(or_1_out));
  Transistor #(.\type ("n")) transistor_131 (.in(1'b0), .out(x21), .gate(IR7));
  Transistor #(.\type ("n")) transistor_132 (.in(1'b0), .out(x21), .gate(IR4));
  Transistor #(.\type ("n")) transistor_133 (.in(1'b0), .out(x21), .gate(IR3));
  Transistor #(.\type ("n")) transistor_134 (.in(1'b0), .out(x21), .gate(IR2));
  Transistor #(.\type ("n")) transistor_135 (.in(1'b0), .out(x21), .gate(IR6));
  Transistor #(.\type ("n")) transistor_136 (.in(1'b0), .out(x21), .gate(not_8_out));
  Transistor #(.\type ("n")) transistor_137 (.in(1'b0), .out(x21), .gate(n_T0));
  Pull_Resistor #(.pull(1)) pull_resistor_23 (.node(x22));
  Transistor #(.\type ("n")) transistor_138 (.in(1'b0), .out(x22), .gate(n_T5));
  Transistor #(.\type ("n")) transistor_139 (.in(1'b0), .out(x22), .gate(or_1_out));
  Transistor #(.\type ("n")) transistor_140 (.in(1'b0), .out(x22), .gate(IR7));
  Transistor #(.\type ("n")) transistor_141 (.in(1'b0), .out(x22), .gate(IR4));
  Transistor #(.\type ("n")) transistor_142 (.in(1'b0), .out(x22), .gate(IR3));
  Transistor #(.\type ("n")) transistor_143 (.in(1'b0), .out(x22), .gate(IR2));
  Transistor #(.\type ("n")) transistor_144 (.in(1'b0), .out(x22), .gate(IR6));
  Transistor #(.\type ("n")) transistor_145 (.in(1'b0), .out(x22), .gate(IR5));
  Pull_Resistor #(.pull(1)) pull_resistor_24 (.node(x23));
  Transistor #(.\type ("n")) transistor_146 (.in(1'b0), .out(x23), .gate(or_1_out));
  Transistor #(.\type ("n")) transistor_147 (.in(1'b0), .out(x23), .gate(IR7));
  Transistor #(.\type ("n")) transistor_148 (.in(1'b0), .out(x23), .gate(IR4));
  Transistor #(.\type ("n")) transistor_149 (.in(1'b0), .out(x23), .gate(not_5_out));
  Transistor #(.\type ("n")) transistor_150 (.in(1'b0), .out(x23), .gate(IR2));
  Transistor #(.\type ("n")) transistor_151 (.in(1'b0), .out(x23), .gate(IR5));
  Transistor #(.\type ("n")) transistor_152 (.in(1'b0), .out(x23), .gate(n_T0));
  Pull_Resistor #(.pull(1)) pull_resistor_25 (.node(x24));
  Pull_Resistor #(.pull(1)) pull_resistor_26 (.node(x25));
  Transistor #(.\type ("n")) transistor_153 (.in(1'b0), .out(x24), .gate(n_T4));
  Transistor #(.\type ("n")) transistor_154 (.in(1'b0), .out(x25), .gate(n_T3));
  Transistor #(.\type ("n")) transistor_155 (.in(1'b0), .out(x24), .gate(or_1_out));
  Transistor #(.\type ("n")) transistor_156 (.in(1'b0), .out(x25), .gate(or_1_out));
  Transistor #(.\type ("n")) transistor_157 (.in(1'b0), .out(x24), .gate(IR7));
  Transistor #(.\type ("n")) transistor_158 (.in(1'b0), .out(x25), .gate(IR7));
  Transistor #(.\type ("n")) transistor_159 (.in(1'b0), .out(x24), .gate(IR4));
  Transistor #(.\type ("n")) transistor_160 (.in(1'b0), .out(x25), .gate(IR4));
  Transistor #(.\type ("n")) transistor_161 (.in(1'b0), .out(x24), .gate(IR3));
  Transistor #(.\type ("n")) transistor_162 (.in(1'b0), .out(x25), .gate(not_5_out));
  Transistor #(.\type ("n")) transistor_163 (.in(1'b0), .out(x24), .gate(IR2));
  Transistor #(.\type ("n")) transistor_164 (.in(1'b0), .out(x25), .gate(IR2));
  Transistor #(.\type ("n")) transistor_165 (.in(1'b0), .out(x24), .gate(not_7_out));
  Transistor #(.\type ("n")) transistor_166 (.in(1'b0), .out(x24), .gate(not_8_out));
  Transistor #(.\type ("n")) transistor_167 (.in(1'b0), .out(x25), .gate(not_8_out));
  Pull_Resistor #(.pull(1)) pull_resistor_27 (.node(x26));
  Transistor #(.\type ("n")) transistor_168 (.in(1'b0), .out(x26), .gate(n_T5));
  Transistor #(.\type ("n")) transistor_169 (.in(1'b0), .out(x26), .gate(or_1_out));
  Transistor #(.\type ("n")) transistor_170 (.in(1'b0), .out(x26), .gate(IR7));
  Transistor #(.\type ("n")) transistor_171 (.in(1'b0), .out(x26), .gate(IR4));
  Transistor #(.\type ("n")) transistor_172 (.in(1'b0), .out(x26), .gate(IR3));
  Transistor #(.\type ("n")) transistor_173 (.in(1'b0), .out(x26), .gate(IR2));
  Transistor #(.\type ("n")) transistor_174 (.in(1'b0), .out(x26), .gate(not_7_out));
  Transistor #(.\type ("n")) transistor_175 (.in(1'b0), .out(x26), .gate(IR5));
  Pull_Resistor #(.pull(1)) pull_resistor_28 (.node(x27));
  Transistor #(.\type ("n")) transistor_176 (.in(1'b0), .out(x27), .gate(not_1_out));
  Transistor #(.\type ("n")) transistor_177 (.in(1'b0), .out(x27), .gate(IR7));
  Transistor #(.\type ("n")) transistor_178 (.in(1'b0), .out(x27), .gate(not_7_out));
  Transistor #(.\type ("n")) transistor_179 (.in(1'b0), .out(x27), .gate(not_8_out));
  Pull_Resistor #(.pull(1)) pull_resistor_29 (.node(x28));
  Pull_Resistor #(.pull(1)) pull_resistor_30 (.node(x29));
  Transistor #(.\type ("n")) transistor_180 (.in(1'b0), .out(x28), .gate(n_T2));
  Transistor #(.\type ("n")) transistor_181 (.in(1'b0), .out(x29), .gate(not_2_out));
  Transistor #(.\type ("n")) transistor_182 (.in(1'b0), .out(x29), .gate(IR7));
  Transistor #(.\type ("n")) transistor_183 (.in(1'b0), .out(x29), .gate(not_7_out));
  Transistor #(.\type ("n")) transistor_184 (.in(1'b0), .out(x29), .gate(IR5));
  Transistor #(.\type ("n")) transistor_185 (.in(1'b0), .out(x29), .gate(n_T0));
  Pull_Resistor #(.pull(1)) pull_resistor_31 (.node(x30));
  Transistor #(.\type ("n")) transistor_186 (.in(1'b0), .out(x30), .gate(or_1_out));
  Transistor #(.\type ("n")) transistor_187 (.in(1'b0), .out(x30), .gate(IR7));
  Transistor #(.\type ("n")) transistor_188 (.in(1'b0), .out(x30), .gate(IR4));
  Transistor #(.\type ("n")) transistor_189 (.in(1'b0), .out(x30), .gate(not_5_out));
  Transistor #(.\type ("n")) transistor_190 (.in(1'b0), .out(x30), .gate(not_6_out));
  Transistor #(.\type ("n")) transistor_191 (.in(1'b0), .out(x30), .gate(not_7_out));
  Pull_Resistor #(.pull(1)) pull_resistor_32 (.node(x31));
  Transistor #(.\type ("n")) transistor_192 (.in(1'b0), .out(x31), .gate(n_T2));
  Transistor #(.\type ("n")) transistor_193 (.in(1'b0), .out(x31), .gate(IR4));
  Transistor #(.\type ("n")) transistor_194 (.in(1'b0), .out(x31), .gate(not_5_out));
  Transistor #(.\type ("n")) transistor_195 (.in(1'b0), .out(x31), .gate(not_6_out));
  Pull_Resistor #(.pull(1)) pull_resistor_33 (.node(x32));
  Pull_Resistor #(.pull(1)) pull_resistor_34 (.node(x33));
  Transistor #(.\type ("n")) transistor_196 (.in(1'b0), .out(x33), .gate(n_T2));
  Transistor #(.\type ("n")) transistor_197 (.in(1'b0), .out(x32), .gate(not_2_out));
  Transistor #(.\type ("n")) transistor_198 (.in(1'b0), .out(x32), .gate(IR7));
  Transistor #(.\type ("n")) transistor_199 (.in(1'b0), .out(x33), .gate(IR3));
  Transistor #(.\type ("n")) transistor_200 (.in(1'b0), .out(x32), .gate(IR6));
  Transistor #(.\type ("n")) transistor_201 (.in(1'b0), .out(x32), .gate(IR5));
  Transistor #(.\type ("n")) transistor_202 (.in(1'b0), .out(x32), .gate(n_T0));
  Pull_Resistor #(.pull(1)) pull_resistor_35 (.node(x34));
  Transistor #(.\type ("n")) transistor_203 (.in(1'b0), .out(x34), .gate(n_T0));
  Pull_Resistor #(.pull(1)) pull_resistor_36 (.node(x35));
  Transistor #(.\type ("n")) transistor_204 (.in(1'b0), .out(x35), .gate(n_T2));
  Transistor #(.\type ("n")) transistor_205 (.in(1'b0), .out(x35), .gate(or_1_out));
  Transistor #(.\type ("n")) transistor_206 (.in(1'b0), .out(x35), .gate(IR7));
  Transistor #(.\type ("n")) transistor_207 (.in(1'b0), .out(x35), .gate(IR4));
  Transistor #(.\type ("n")) transistor_208 (.in(1'b0), .out(x35), .gate(IR2));
  Pull_Resistor #(.pull(1)) pull_resistor_37 (.node(x36));
  Transistor #(.\type ("n")) transistor_209 (.in(1'b0), .out(x36), .gate(n_T3));
  Transistor #(.\type ("n")) transistor_210 (.in(1'b0), .out(x36), .gate(or_1_out));
  Transistor #(.\type ("n")) transistor_211 (.in(1'b0), .out(x36), .gate(IR7));
  Transistor #(.\type ("n")) transistor_212 (.in(1'b0), .out(x36), .gate(IR4));
  Pull_Resistor #(.pull(1)) pull_resistor_38 (.node(x37));
  Transistor #(.\type ("n")) transistor_213 (.in(1'b0), .out(x37), .gate(n_T4));
  Transistor #(.\type ("n")) transistor_214 (.in(1'b0), .out(x37), .gate(or_1_out));
  Transistor #(.\type ("n")) transistor_215 (.in(1'b0), .out(x37), .gate(IR7));
  Transistor #(.\type ("n")) transistor_216 (.in(1'b0), .out(x37), .gate(IR4));
  Transistor #(.\type ("n")) transistor_217 (.in(1'b0), .out(x37), .gate(IR3));
  Transistor #(.\type ("n")) transistor_218 (.in(1'b0), .out(x37), .gate(IR2));
  Transistor #(.\type ("n")) transistor_219 (.in(1'b0), .out(x37), .gate(IR6));
  Pull_Resistor #(.pull(1)) pull_resistor_39 (.node(x38));
  Transistor #(.\type ("n")) transistor_220 (.in(1'b0), .out(x38), .gate(n_T4));
  Transistor #(.\type ("n")) transistor_221 (.in(1'b0), .out(x38), .gate(or_1_out));
  Transistor #(.\type ("n")) transistor_222 (.in(1'b0), .out(x38), .gate(IR7));
  Transistor #(.\type ("n")) transistor_223 (.in(1'b0), .out(x38), .gate(IR4));
  Transistor #(.\type ("n")) transistor_224 (.in(1'b0), .out(x38), .gate(IR3));
  Transistor #(.\type ("n")) transistor_225 (.in(1'b0), .out(x38), .gate(IR2));
  Transistor #(.\type ("n")) transistor_226 (.in(1'b0), .out(x38), .gate(not_7_out));
  Transistor #(.\type ("n")) transistor_227 (.in(1'b0), .out(x38), .gate(IR5));
  Pull_Resistor #(.pull(1)) pull_resistor_40 (.node(x39));
  Pull_Resistor #(.pull(1)) pull_resistor_41 (.node(x40));
  Transistor #(.\type ("n")) transistor_228 (.in(1'b0), .out(x40), .gate(n_T4));
  Transistor #(.\type ("n")) transistor_229 (.in(1'b0), .out(x39), .gate(n_T3));
  Transistor #(.\type ("n")) transistor_230 (.in(1'b0), .out(x39), .gate(not_2_out));
  Transistor #(.\type ("n")) transistor_231 (.in(1'b0), .out(x40), .gate(not_2_out));
  Transistor #(.\type ("n")) transistor_232 (.in(1'b0), .out(x39), .gate(IR4));
  Transistor #(.\type ("n")) transistor_233 (.in(1'b0), .out(x40), .gate(not_4_out));
  Transistor #(.\type ("n")) transistor_234 (.in(1'b0), .out(x39), .gate(IR3));
  Transistor #(.\type ("n")) transistor_235 (.in(1'b0), .out(x40), .gate(IR3));
  Transistor #(.\type ("n")) transistor_236 (.in(1'b0), .out(x39), .gate(IR2));
  Transistor #(.\type ("n")) transistor_237 (.in(1'b0), .out(x40), .gate(IR2));
  Pull_Resistor #(.pull(1)) pull_resistor_42 (.node(x41));
  Transistor #(.\type ("n")) transistor_238 (.in(1'b0), .out(x41), .gate(n_T2));
  Transistor #(.\type ("n")) transistor_239 (.in(1'b0), .out(x41), .gate(not_2_out));
  Transistor #(.\type ("n")) transistor_240 (.in(1'b0), .out(x41), .gate(not_4_out));
  Transistor #(.\type ("n")) transistor_241 (.in(1'b0), .out(x41), .gate(IR3));
  Transistor #(.\type ("n")) transistor_242 (.in(1'b0), .out(x41), .gate(IR2));
  Pull_Resistor #(.pull(1)) pull_resistor_43 (.node(x42));
  Transistor #(.\type ("n")) transistor_243 (.in(1'b0), .out(x42), .gate(n_T3));
  Transistor #(.\type ("n")) transistor_244 (.in(1'b0), .out(x42), .gate(not_4_out));
  Transistor #(.\type ("n")) transistor_245 (.in(1'b0), .out(x42), .gate(not_5_out));
  Pull_Resistor #(.pull(1)) pull_resistor_44 (.node(x43));
  Pull_Resistor #(.pull(1)) pull_resistor_45 (.node(x44));
  Transistor #(.\type ("n")) transistor_246 (.in(1'b0), .out(x44), .gate(not_1_out));
  Transistor #(.\type ("n")) transistor_247 (.in(1'b0), .out(x43), .gate(or_1_out));
  Transistor #(.\type ("n")) transistor_248 (.in(1'b0), .out(x43), .gate(IR7));
  Transistor #(.\type ("n")) transistor_249 (.in(1'b0), .out(x44), .gate(not_3_out));
  Transistor #(.\type ("n")) transistor_250 (.in(1'b0), .out(x43), .gate(IR4));
  Transistor #(.\type ("n")) transistor_251 (.in(1'b0), .out(x43), .gate(not_5_out));
  Transistor #(.\type ("n")) transistor_252 (.in(1'b0), .out(x43), .gate(IR2));
  Transistor #(.\type ("n")) transistor_253 (.in(1'b0), .out(x44), .gate(not_7_out));
  Transistor #(.\type ("n")) transistor_254 (.in(1'b0), .out(x43), .gate(not_8_out));
  Transistor #(.\type ("n")) transistor_255 (.in(1'b0), .out(x44), .gate(not_8_out));
  Pull_Resistor #(.pull(1)) pull_resistor_46 (.node(x45));
  Transistor #(.\type ("n")) transistor_256 (.in(1'b0), .out(x45), .gate(n_T4));
  Transistor #(.\type ("n")) transistor_257 (.in(1'b0), .out(x45), .gate(not_2_out));
  Transistor #(.\type ("n")) transistor_258 (.in(1'b0), .out(x45), .gate(IR4));
  Transistor #(.\type ("n")) transistor_259 (.in(1'b0), .out(x45), .gate(IR3));
  Transistor #(.\type ("n")) transistor_260 (.in(1'b0), .out(x45), .gate(IR2));
  Pull_Resistor #(.pull(1)) pull_resistor_47 (.node(x46));
  Transistor #(.\type ("n")) transistor_261 (.in(1'b0), .out(x46), .gate(n_T3));
  Transistor #(.\type ("n")) transistor_262 (.in(1'b0), .out(x46), .gate(not_2_out));
  Transistor #(.\type ("n")) transistor_263 (.in(1'b0), .out(x46), .gate(not_4_out));
  Transistor #(.\type ("n")) transistor_264 (.in(1'b0), .out(x46), .gate(IR3));
  Transistor #(.\type ("n")) transistor_265 (.in(1'b0), .out(x46), .gate(IR2));
  Pull_Resistor #(.pull(1)) pull_resistor_48 (.node(x47));
  Pull_Resistor #(.pull(1)) pull_resistor_49 (.node(x48));
  Transistor #(.\type ("n")) transistor_266 (.in(1'b0), .out(x48), .gate(n_T2));
  Transistor #(.\type ("n")) transistor_267 (.in(1'b0), .out(x47), .gate(or_1_out));
  Transistor #(.\type ("n")) transistor_268 (.in(1'b0), .out(x48), .gate(or_1_out));
  Transistor #(.\type ("n")) transistor_269 (.in(1'b0), .out(x47), .gate(IR7));
  Transistor #(.\type ("n")) transistor_270 (.in(1'b0), .out(x48), .gate(IR7));
  Transistor #(.\type ("n")) transistor_271 (.in(1'b0), .out(x47), .gate(IR4));
  Transistor #(.\type ("n")) transistor_272 (.in(1'b0), .out(x48), .gate(IR4));
  Transistor #(.\type ("n")) transistor_273 (.in(1'b0), .out(x47), .gate(IR3));
  Transistor #(.\type ("n")) transistor_274 (.in(1'b0), .out(x48), .gate(IR3));
  Transistor #(.\type ("n")) transistor_275 (.in(1'b0), .out(x47), .gate(IR2));
  Transistor #(.\type ("n")) transistor_276 (.in(1'b0), .out(x48), .gate(IR2));
  Transistor #(.\type ("n")) transistor_277 (.in(1'b0), .out(x48), .gate(IR6));
  Transistor #(.\type ("n")) transistor_278 (.in(1'b0), .out(x47), .gate(not_7_out));
  Transistor #(.\type ("n")) transistor_279 (.in(1'b0), .out(x48), .gate(not_8_out));
  Pull_Resistor #(.pull(1)) pull_resistor_50 (.node(x49));
  Transistor #(.\type ("n")) transistor_280 (.in(1'b0), .out(x49), .gate(or_1_out));
  Transistor #(.\type ("n")) transistor_281 (.in(1'b0), .out(x49), .gate(not_3_out));
  Transistor #(.\type ("n")) transistor_282 (.in(1'b0), .out(x49), .gate(IR4));
  Transistor #(.\type ("n")) transistor_283 (.in(1'b0), .out(x49), .gate(not_7_out));
  Transistor #(.\type ("n")) transistor_284 (.in(1'b0), .out(x49), .gate(n_T0));
  Pull_Resistor #(.pull(1)) pull_resistor_51 (.node(x50));
  Transistor #(.\type ("n")) transistor_285 (.in(1'b0), .out(x50), .gate(not_2_out));
  Transistor #(.\type ("n")) transistor_286 (.in(1'b0), .out(x50), .gate(not_3_out));
  Transistor #(.\type ("n")) transistor_287 (.in(1'b0), .out(x50), .gate(not_7_out));
  Transistor #(.\type ("n")) transistor_288 (.in(1'b0), .out(x50), .gate(IR5));
  Transistor #(.\type ("n")) transistor_289 (.in(1'b0), .out(x50), .gate(n_T0));
  Pull_Resistor #(.pull(1)) pull_resistor_52 (.node(x51));
  Pull_Resistor #(.pull(1)) pull_resistor_53 (.node(x52));
  Transistor #(.\type ("n")) transistor_290 (.in(1'b0), .out(x51), .gate(not_2_out));
  Transistor #(.\type ("n")) transistor_291 (.in(1'b0), .out(x52), .gate(not_2_out));
  Transistor #(.\type ("n")) transistor_292 (.in(1'b0), .out(x51), .gate(not_3_out));
  Transistor #(.\type ("n")) transistor_293 (.in(1'b0), .out(x51), .gate(not_7_out));
  Transistor #(.\type ("n")) transistor_294 (.in(1'b0), .out(x52), .gate(not_7_out));
  Transistor #(.\type ("n")) transistor_295 (.in(1'b0), .out(x51), .gate(not_8_out));
  Transistor #(.\type ("n")) transistor_296 (.in(1'b0), .out(x52), .gate(not_8_out));
  Transistor #(.\type ("n")) transistor_297 (.in(1'b0), .out(x51), .gate(n_T0));
  Transistor #(.\type ("n")) transistor_298 (.in(1'b0), .out(x52), .gate(n_T0));
  Pull_Resistor #(.pull(1)) pull_resistor_54 (.node(x53));
  Transistor #(.\type ("n")) transistor_299 (.in(1'b0), .out(x53), .gate(not_1_out));
  Transistor #(.\type ("n")) transistor_300 (.in(1'b0), .out(x53), .gate(IR7));
  Transistor #(.\type ("n")) transistor_301 (.in(1'b0), .out(x53), .gate(IR6));
  Transistor #(.\type ("n")) transistor_302 (.in(1'b0), .out(x53), .gate(not_8_out));
  Pull_Resistor #(.pull(1)) pull_resistor_55 (.node(x54));
  Transistor #(.\type ("n")) transistor_303 (.in(1'b0), .out(x54), .gate(n_T3));
  Transistor #(.\type ("n")) transistor_304 (.in(1'b0), .out(x54), .gate(or_1_out));
  Transistor #(.\type ("n")) transistor_305 (.in(1'b0), .out(x54), .gate(IR7));
  Transistor #(.\type ("n")) transistor_306 (.in(1'b0), .out(x54), .gate(IR4));
  Transistor #(.\type ("n")) transistor_307 (.in(1'b0), .out(x54), .gate(not_5_out));
  Transistor #(.\type ("n")) transistor_308 (.in(1'b0), .out(x54), .gate(not_6_out));
  Transistor #(.\type ("n")) transistor_309 (.in(1'b0), .out(x54), .gate(not_7_out));
  Pull_Resistor #(.pull(1)) pull_resistor_56 (.node(x55));
  Pull_Resistor #(.pull(1)) pull_resistor_57 (.node(x56));
  Transistor #(.\type ("n")) transistor_310 (.in(1'b0), .out(x56), .gate(n_T5));
  Transistor #(.\type ("n")) transistor_311 (.in(1'b0), .out(x55), .gate(not_1_out));
  Transistor #(.\type ("n")) transistor_312 (.in(1'b0), .out(x56), .gate(or_1_out));
  Transistor #(.\type ("n")) transistor_313 (.in(1'b0), .out(x55), .gate(IR7));
  Transistor #(.\type ("n")) transistor_314 (.in(1'b0), .out(x56), .gate(IR7));
  Transistor #(.\type ("n")) transistor_315 (.in(1'b0), .out(x56), .gate(IR4));
  Transistor #(.\type ("n")) transistor_316 (.in(1'b0), .out(x56), .gate(IR3));
  Transistor #(.\type ("n")) transistor_317 (.in(1'b0), .out(x56), .gate(IR2));
  Transistor #(.\type ("n")) transistor_318 (.in(1'b0), .out(x55), .gate(IR6));
  Transistor #(.\type ("n")) transistor_319 (.in(1'b0), .out(x56), .gate(IR6));
  Transistor #(.\type ("n")) transistor_320 (.in(1'b0), .out(x56), .gate(not_8_out));
  Pull_Resistor #(.pull(1)) pull_resistor_58 (.node(x57));
  Transistor #(.\type ("n")) transistor_321 (.in(1'b0), .out(x57), .gate(n_T2));
  Transistor #(.\type ("n")) transistor_322 (.in(1'b0), .out(x57), .gate(or_1_out));
  Transistor #(.\type ("n")) transistor_323 (.in(1'b0), .out(x57), .gate(IR7));
  Transistor #(.\type ("n")) transistor_324 (.in(1'b0), .out(x57), .gate(IR4));
  Transistor #(.\type ("n")) transistor_325 (.in(1'b0), .out(x57), .gate(IR2));
  Pull_Resistor #(.pull(1)) pull_resistor_59 (.node(x58));
  Transistor #(.\type ("n")) transistor_326 (.in(1'b0), .out(x58), .gate(or_1_out));
  Transistor #(.\type ("n")) transistor_327 (.in(1'b0), .out(x58), .gate(not_3_out));
  Transistor #(.\type ("n")) transistor_328 (.in(1'b0), .out(x58), .gate(not_4_out));
  Transistor #(.\type ("n")) transistor_329 (.in(1'b0), .out(x58), .gate(not_5_out));
  Transistor #(.\type ("n")) transistor_330 (.in(1'b0), .out(x58), .gate(IR2));
  Transistor #(.\type ("n")) transistor_331 (.in(1'b0), .out(x58), .gate(IR6));
  Transistor #(.\type ("n")) transistor_332 (.in(1'b0), .out(x58), .gate(IR5));
  Transistor #(.\type ("n")) transistor_333 (.in(1'b0), .out(x58), .gate(n_T0));
  Pull_Resistor #(.pull(1)) pull_resistor_60 (.node(x59));
  Pull_Resistor #(.pull(1)) pull_resistor_61 (.node(x60));
  Transistor #(.\type ("n")) transistor_334 (.in(1'b0), .out(x59), .gate(not_2_out));
  Transistor #(.\type ("n")) transistor_335 (.in(1'b0), .out(x60), .gate(not_2_out));
  Transistor #(.\type ("n")) transistor_336 (.in(1'b0), .out(x59), .gate(IR7));
  Transistor #(.\type ("n")) transistor_337 (.in(1'b0), .out(x60), .gate(not_7_out));
  Transistor #(.\type ("n")) transistor_338 (.in(1'b0), .out(x60), .gate(not_8_out));
  Transistor #(.\type ("n")) transistor_339 (.in(1'b0), .out(x59), .gate(n_T1X));
  Transistor #(.\type ("n")) transistor_340 (.in(1'b0), .out(x60), .gate(n_T1X));
  Pull_Resistor #(.pull(1)) pull_resistor_62 (.node(x61));
  Transistor #(.\type ("n")) transistor_341 (.in(1'b0), .out(x61), .gate(not_1_out));
  Transistor #(.\type ("n")) transistor_342 (.in(1'b0), .out(x61), .gate(IR7));
  Transistor #(.\type ("n")) transistor_343 (.in(1'b0), .out(x61), .gate(IR4));
  Transistor #(.\type ("n")) transistor_344 (.in(1'b0), .out(x61), .gate(not_5_out));
  Transistor #(.\type ("n")) transistor_345 (.in(1'b0), .out(x61), .gate(IR2));
  Transistor #(.\type ("n")) transistor_346 (.in(1'b0), .out(x61), .gate(n_T1X));
  Pull_Resistor #(.pull(1)) pull_resistor_63 (.node(x62));
  Transistor #(.\type ("n")) transistor_347 (.in(1'b0), .out(x62), .gate(not_1_out));
  Transistor #(.\type ("n")) transistor_348 (.in(1'b0), .out(x62), .gate(not_3_out));
  Transistor #(.\type ("n")) transistor_349 (.in(1'b0), .out(x62), .gate(IR4));
  Transistor #(.\type ("n")) transistor_350 (.in(1'b0), .out(x62), .gate(not_5_out));
  Transistor #(.\type ("n")) transistor_351 (.in(1'b0), .out(x62), .gate(IR2));
  Transistor #(.\type ("n")) transistor_352 (.in(1'b0), .out(x62), .gate(IR6));
  Transistor #(.\type ("n")) transistor_353 (.in(1'b0), .out(x62), .gate(IR5));
  Transistor #(.\type ("n")) transistor_354 (.in(1'b0), .out(x62), .gate(n_T0));
  Pull_Resistor #(.pull(1)) pull_resistor_64 (.node(x63));
  Pull_Resistor #(.pull(1)) pull_resistor_65 (.node(x64));
  Transistor #(.\type ("n")) transistor_355 (.in(1'b0), .out(x63), .gate(or_1_out));
  Transistor #(.\type ("n")) transistor_356 (.in(1'b0), .out(x64), .gate(not_2_out));
  Transistor #(.\type ("n")) transistor_357 (.in(1'b0), .out(x63), .gate(IR7));
  Transistor #(.\type ("n")) transistor_358 (.in(1'b0), .out(x64), .gate(not_3_out));
  Transistor #(.\type ("n")) transistor_359 (.in(1'b0), .out(x63), .gate(IR4));
  Transistor #(.\type ("n")) transistor_360 (.in(1'b0), .out(x63), .gate(not_5_out));
  Transistor #(.\type ("n")) transistor_361 (.in(1'b0), .out(x63), .gate(IR2));
  Transistor #(.\type ("n")) transistor_362 (.in(1'b0), .out(x64), .gate(IR6));
  Transistor #(.\type ("n")) transistor_363 (.in(1'b0), .out(x63), .gate(not_7_out));
  Transistor #(.\type ("n")) transistor_364 (.in(1'b0), .out(x63), .gate(not_8_out));
  Transistor #(.\type ("n")) transistor_365 (.in(1'b0), .out(x64), .gate(not_8_out));
  Transistor #(.\type ("n")) transistor_366 (.in(1'b0), .out(x63), .gate(n_T0));
  Transistor #(.\type ("n")) transistor_367 (.in(1'b0), .out(x64), .gate(n_T0));
  Pull_Resistor #(.pull(1)) pull_resistor_66 (.node(x65));
  Transistor #(.\type ("n")) transistor_368 (.in(1'b0), .out(x65), .gate(not_2_out));
  Transistor #(.\type ("n")) transistor_369 (.in(1'b0), .out(x65), .gate(n_T0));
  Pull_Resistor #(.pull(1)) pull_resistor_67 (.node(x66));
  Transistor #(.\type ("n")) transistor_370 (.in(1'b0), .out(x66), .gate(or_1_out));
  Transistor #(.\type ("n")) transistor_371 (.in(1'b0), .out(x66), .gate(not_3_out));
  Transistor #(.\type ("n")) transistor_372 (.in(1'b0), .out(x66), .gate(IR4));
  Transistor #(.\type ("n")) transistor_373 (.in(1'b0), .out(x66), .gate(not_5_out));
  Transistor #(.\type ("n")) transistor_374 (.in(1'b0), .out(x66), .gate(IR2));
  Transistor #(.\type ("n")) transistor_375 (.in(1'b0), .out(x66), .gate(IR6));
  Transistor #(.\type ("n")) transistor_376 (.in(1'b0), .out(x66), .gate(not_8_out));
  Transistor #(.\type ("n")) transistor_377 (.in(1'b0), .out(x66), .gate(n_T0));
  Pull_Resistor #(.pull(1)) pull_resistor_68 (.node(x67));
  Pull_Resistor #(.pull(1)) pull_resistor_69 (.node(x68));
  Transistor #(.\type ("n")) transistor_378 (.in(1'b0), .out(x67), .gate(not_1_out));
  Transistor #(.\type ("n")) transistor_379 (.in(1'b0), .out(x68), .gate(not_1_out));
  Transistor #(.\type ("n")) transistor_380 (.in(1'b0), .out(x67), .gate(IR7));
  Transistor #(.\type ("n")) transistor_381 (.in(1'b0), .out(x68), .gate(not_3_out));
  Transistor #(.\type ("n")) transistor_382 (.in(1'b0), .out(x67), .gate(IR4));
  Transistor #(.\type ("n")) transistor_383 (.in(1'b0), .out(x68), .gate(IR4));
  Transistor #(.\type ("n")) transistor_384 (.in(1'b0), .out(x67), .gate(not_5_out));
  Transistor #(.\type ("n")) transistor_385 (.in(1'b0), .out(x68), .gate(not_5_out));
  Transistor #(.\type ("n")) transistor_386 (.in(1'b0), .out(x67), .gate(IR2));
  Transistor #(.\type ("n")) transistor_387 (.in(1'b0), .out(x68), .gate(IR2));
  Transistor #(.\type ("n")) transistor_388 (.in(1'b0), .out(x68), .gate(IR6));
  Transistor #(.\type ("n")) transistor_389 (.in(1'b0), .out(x68), .gate(not_8_out));
  Transistor #(.\type ("n")) transistor_390 (.in(1'b0), .out(x67), .gate(n_T0));
  Transistor #(.\type ("n")) transistor_391 (.in(1'b0), .out(x68), .gate(n_T0));
  Pull_Resistor #(.pull(1)) pull_resistor_70 (.node(x69));
  Transistor #(.\type ("n")) transistor_392 (.in(1'b0), .out(x69), .gate(or_1_out));
  Transistor #(.\type ("n")) transistor_393 (.in(1'b0), .out(x69), .gate(IR7));
  Transistor #(.\type ("n")) transistor_394 (.in(1'b0), .out(x69), .gate(IR4));
  Transistor #(.\type ("n")) transistor_395 (.in(1'b0), .out(x69), .gate(not_6_out));
  Transistor #(.\type ("n")) transistor_396 (.in(1'b0), .out(x69), .gate(IR6));
  Transistor #(.\type ("n")) transistor_397 (.in(1'b0), .out(x69), .gate(not_8_out));
  Transistor #(.\type ("n")) transistor_398 (.in(1'b0), .out(x69), .gate(n_T0));
  Pull_Resistor #(.pull(1)) pull_resistor_71 (.node(x70));
  Transistor #(.\type ("n")) transistor_399 (.in(1'b0), .out(x70), .gate(not_2_out));
  Transistor #(.\type ("n")) transistor_400 (.in(1'b0), .out(x70), .gate(IR7));
  Transistor #(.\type ("n")) transistor_401 (.in(1'b0), .out(x70), .gate(IR6));
  Transistor #(.\type ("n")) transistor_402 (.in(1'b0), .out(x70), .gate(not_8_out));
  Transistor #(.\type ("n")) transistor_403 (.in(1'b0), .out(x70), .gate(n_T0));
  Pull_Resistor #(.pull(1)) pull_resistor_72 (.node(x71));
  Pull_Resistor #(.pull(1)) pull_resistor_73 (.node(x72));
  Transistor #(.\type ("n")) transistor_404 (.in(1'b0), .out(x72), .gate(n_T5));
  Transistor #(.\type ("n")) transistor_405 (.in(1'b0), .out(x71), .gate(n_T4));
  Transistor #(.\type ("n")) transistor_406 (.in(1'b0), .out(x72), .gate(not_2_out));
  Transistor #(.\type ("n")) transistor_407 (.in(1'b0), .out(x71), .gate(not_4_out));
  Transistor #(.\type ("n")) transistor_408 (.in(1'b0), .out(x72), .gate(not_4_out));
  Transistor #(.\type ("n")) transistor_409 (.in(1'b0), .out(x72), .gate(IR3));
  Transistor #(.\type ("n")) transistor_410 (.in(1'b0), .out(x71), .gate(not_5_out));
  Transistor #(.\type ("n")) transistor_411 (.in(1'b0), .out(x72), .gate(IR2));
  Pull_Resistor #(.pull(1)) pull_resistor_74 (.node(x73));
  Transistor #(.\type ("n")) transistor_412 (.in(1'b0), .out(x73), .gate(or_1_out));
  Transistor #(.\type ("n")) transistor_413 (.in(1'b0), .out(x73), .gate(not_4_out));
  Transistor #(.\type ("n")) transistor_414 (.in(1'b0), .out(x73), .gate(IR3));
  Transistor #(.\type ("n")) transistor_415 (.in(1'b0), .out(x73), .gate(IR2));
  Transistor #(.\type ("n")) transistor_416 (.in(1'b0), .out(x73), .gate(n_T0));
  Pull_Resistor #(.pull(1)) pull_resistor_75 (.node(x74));
  Pull_Resistor #(.pull(1)) pull_resistor_76 (.node(x75));
  Transistor #(.\type ("n")) transistor_417 (.in(1'b0), .out(x74), .gate(n_T2));
  Transistor #(.\type ("n")) transistor_418 (.in(1'b0), .out(x75), .gate(not_1_out));
  Transistor #(.\type ("n")) transistor_419 (.in(1'b0), .out(x74), .gate(or_1_out));
  Transistor #(.\type ("n")) transistor_420 (.in(1'b0), .out(x74), .gate(IR7));
  Transistor #(.\type ("n")) transistor_421 (.in(1'b0), .out(x75), .gate(IR7));
  Transistor #(.\type ("n")) transistor_422 (.in(1'b0), .out(x74), .gate(IR4));
  Transistor #(.\type ("n")) transistor_423 (.in(1'b0), .out(x75), .gate(IR4));
  Transistor #(.\type ("n")) transistor_424 (.in(1'b0), .out(x74), .gate(not_5_out));
  Transistor #(.\type ("n")) transistor_425 (.in(1'b0), .out(x75), .gate(not_5_out));
  Transistor #(.\type ("n")) transistor_426 (.in(1'b0), .out(x74), .gate(IR2));
  Transistor #(.\type ("n")) transistor_427 (.in(1'b0), .out(x75), .gate(IR2));
  Transistor #(.\type ("n")) transistor_428 (.in(1'b0), .out(x74), .gate(not_7_out));
  Transistor #(.\type ("n")) transistor_429 (.in(1'b0), .out(x75), .gate(not_7_out));
  Transistor #(.\type ("n")) transistor_430 (.in(1'b0), .out(x74), .gate(IR5));
  Transistor #(.\type ("n")) transistor_431 (.in(1'b0), .out(x75), .gate(n_T0));
  Pull_Resistor #(.pull(1)) pull_resistor_77 (.node(x76));
  Transistor #(.\type ("n")) transistor_432 (.in(1'b0), .out(x76), .gate(not_1_out));
  Transistor #(.\type ("n")) transistor_433 (.in(1'b0), .out(x76), .gate(IR7));
  Transistor #(.\type ("n")) transistor_434 (.in(1'b0), .out(x76), .gate(not_7_out));
  Pull_Resistor #(.pull(1)) pull_resistor_78 (.node(x77));
  Transistor #(.\type ("n")) transistor_435 (.in(1'b0), .out(x77), .gate(n_T2));
  Transistor #(.\type ("n")) transistor_436 (.in(1'b0), .out(x77), .gate(or_1_out));
  Transistor #(.\type ("n")) transistor_437 (.in(1'b0), .out(x77), .gate(IR7));
  Transistor #(.\type ("n")) transistor_438 (.in(1'b0), .out(x77), .gate(IR4));
  Transistor #(.\type ("n")) transistor_439 (.in(1'b0), .out(x77), .gate(IR3));
  Transistor #(.\type ("n")) transistor_440 (.in(1'b0), .out(x77), .gate(IR2));
  Transistor #(.\type ("n")) transistor_441 (.in(1'b0), .out(x77), .gate(IR6));
  Transistor #(.\type ("n")) transistor_442 (.in(1'b0), .out(x77), .gate(IR5));
  Pull_Resistor #(.pull(1)) pull_resistor_79 (.node(x78));
  Pull_Resistor #(.pull(1)) pull_resistor_80 (.node(x79));
  Transistor #(.\type ("n")) transistor_443 (.in(1'b0), .out(x78), .gate(n_T3));
  Transistor #(.\type ("n")) transistor_444 (.in(1'b0), .out(x78), .gate(or_1_out));
  Transistor #(.\type ("n")) transistor_445 (.in(1'b0), .out(x79), .gate(not_2_out));
  Transistor #(.\type ("n")) transistor_446 (.in(1'b0), .out(x78), .gate(IR7));
  Transistor #(.\type ("n")) transistor_447 (.in(1'b0), .out(x79), .gate(not_3_out));
  Transistor #(.\type ("n")) transistor_448 (.in(1'b0), .out(x78), .gate(IR4));
  Transistor #(.\type ("n")) transistor_449 (.in(1'b0), .out(x78), .gate(IR3));
  Transistor #(.\type ("n")) transistor_450 (.in(1'b0), .out(x78), .gate(IR2));
  Transistor #(.\type ("n")) transistor_451 (.in(1'b0), .out(x78), .gate(IR6));
  Transistor #(.\type ("n")) transistor_452 (.in(1'b0), .out(x79), .gate(IR6));
  Transistor #(.\type ("n")) transistor_453 (.in(1'b0), .out(x79), .gate(IR5));
  Transistor #(.\type ("n")) transistor_454 (.in(1'b0), .out(x78), .gate(not_8_out));
  Pull_Resistor #(.pull(1)) pull_resistor_81 (.node(x80));
  Transistor #(.\type ("n")) transistor_455 (.in(1'b0), .out(x80), .gate(n_T2));
  Transistor #(.\type ("n")) transistor_456 (.in(1'b0), .out(x80), .gate(or_1_out));
  Transistor #(.\type ("n")) transistor_457 (.in(1'b0), .out(x80), .gate(not_4_out));
  Transistor #(.\type ("n")) transistor_458 (.in(1'b0), .out(x80), .gate(IR3));
  Transistor #(.\type ("n")) transistor_459 (.in(1'b0), .out(x80), .gate(IR2));
  Pull_Resistor #(.pull(1)) pull_resistor_82 (.node(x81));
  Transistor #(.\type ("n")) transistor_460 (.in(1'b0), .out(x81), .gate(n_T2));
  Transistor #(.\type ("n")) transistor_461 (.in(1'b0), .out(x81), .gate(IR3));
  Transistor #(.\type ("n")) transistor_462 (.in(1'b0), .out(x81), .gate(not_6_out));
  Pull_Resistor #(.pull(1)) pull_resistor_83 (.node(x82));
  Pull_Resistor #(.pull(1)) pull_resistor_84 (.node(x83));
  Transistor #(.\type ("n")) transistor_463 (.in(1'b0), .out(x82), .gate(n_T2));
  Transistor #(.\type ("n")) transistor_464 (.in(1'b0), .out(x83), .gate(n_T2));
  Transistor #(.\type ("n")) transistor_465 (.in(1'b0), .out(x82), .gate(not_2_out));
  Transistor #(.\type ("n")) transistor_466 (.in(1'b0), .out(x82), .gate(IR3));
  Transistor #(.\type ("n")) transistor_467 (.in(1'b0), .out(x83), .gate(not_5_out));
  Transistor #(.\type ("n")) transistor_468 (.in(1'b0), .out(x82), .gate(IR2));
  Pull_Resistor #(.pull(1)) pull_resistor_85 (.node(x84));
  Transistor #(.\type ("n")) transistor_469 (.in(1'b0), .out(x84), .gate(n_T5));
  Transistor #(.\type ("n")) transistor_470 (.in(1'b0), .out(x84), .gate(or_1_out));
  Transistor #(.\type ("n")) transistor_471 (.in(1'b0), .out(x84), .gate(IR7));
  Transistor #(.\type ("n")) transistor_472 (.in(1'b0), .out(x84), .gate(IR4));
  Transistor #(.\type ("n")) transistor_473 (.in(1'b0), .out(x84), .gate(IR3));
  Transistor #(.\type ("n")) transistor_474 (.in(1'b0), .out(x84), .gate(IR2));
  Transistor #(.\type ("n")) transistor_475 (.in(1'b0), .out(x84), .gate(not_7_out));
  Transistor #(.\type ("n")) transistor_476 (.in(1'b0), .out(x84), .gate(not_8_out));
  Pull_Resistor #(.pull(1)) pull_resistor_86 (.node(x85));
  Transistor #(.\type ("n")) transistor_477 (.in(1'b0), .out(x85), .gate(n_T4));
  Pull_Resistor #(.pull(1)) pull_resistor_87 (.node(x86));
  Pull_Resistor #(.pull(1)) pull_resistor_88 (.node(x87));
  Transistor #(.\type ("n")) transistor_478 (.in(1'b0), .out(x86), .gate(n_T3));
  Transistor #(.\type ("n")) transistor_479 (.in(1'b0), .out(x87), .gate(or_1_out));
  Transistor #(.\type ("n")) transistor_480 (.in(1'b0), .out(x87), .gate(IR7));
  Transistor #(.\type ("n")) transistor_481 (.in(1'b0), .out(x87), .gate(IR4));
  Transistor #(.\type ("n")) transistor_482 (.in(1'b0), .out(x87), .gate(IR3));
  Transistor #(.\type ("n")) transistor_483 (.in(1'b0), .out(x87), .gate(IR2));
  Transistor #(.\type ("n")) transistor_484 (.in(1'b0), .out(x87), .gate(IR5));
  Transistor #(.\type ("n")) transistor_485 (.in(1'b0), .out(x87), .gate(n_T0));
  Pull_Resistor #(.pull(1)) pull_resistor_89 (.node(x88));
  Transistor #(.\type ("n")) transistor_486 (.in(1'b0), .out(x88), .gate(or_1_out));
  Transistor #(.\type ("n")) transistor_487 (.in(1'b0), .out(x88), .gate(IR7));
  Transistor #(.\type ("n")) transistor_488 (.in(1'b0), .out(x88), .gate(IR4));
  Transistor #(.\type ("n")) transistor_489 (.in(1'b0), .out(x88), .gate(not_5_out));
  Transistor #(.\type ("n")) transistor_490 (.in(1'b0), .out(x88), .gate(not_6_out));
  Transistor #(.\type ("n")) transistor_491 (.in(1'b0), .out(x88), .gate(not_7_out));
  Transistor #(.\type ("n")) transistor_492 (.in(1'b0), .out(x88), .gate(n_T0));
  Pull_Resistor #(.pull(1)) pull_resistor_90 (.node(x89));
  Transistor #(.\type ("n")) transistor_493 (.in(1'b0), .out(x89), .gate(n_T5));
  Transistor #(.\type ("n")) transistor_494 (.in(1'b0), .out(x89), .gate(not_2_out));
  Transistor #(.\type ("n")) transistor_495 (.in(1'b0), .out(x89), .gate(IR4));
  Transistor #(.\type ("n")) transistor_496 (.in(1'b0), .out(x89), .gate(IR3));
  Transistor #(.\type ("n")) transistor_497 (.in(1'b0), .out(x89), .gate(IR2));
  Pull_Resistor #(.pull(1)) pull_resistor_91 (.node(x90));
  Transistor #(.\type ("n")) transistor_498 (.in(1'b0), .out(x90), .gate(n_T3));
  Transistor #(.\type ("n")) transistor_499 (.in(1'b0), .out(x90), .gate(not_5_out));
  Pull_Resistor #(.pull(1)) pull_resistor_92 (.node(x91));
  Transistor #(.\type ("n")) transistor_500 (.in(1'b0), .out(x91), .gate(n_T4));
  Transistor #(.\type ("n")) transistor_501 (.in(1'b0), .out(x91), .gate(not_2_out));
  Transistor #(.\type ("n")) transistor_502 (.in(1'b0), .out(x91), .gate(not_4_out));
  Transistor #(.\type ("n")) transistor_503 (.in(1'b0), .out(x91), .gate(IR3));
  Transistor #(.\type ("n")) transistor_504 (.in(1'b0), .out(x91), .gate(IR2));
  Pull_Resistor #(.pull(1)) pull_resistor_93 (.node(x92));
  Transistor #(.\type ("n")) transistor_505 (.in(1'b0), .out(x92), .gate(n_T3));
  Transistor #(.\type ("n")) transistor_506 (.in(1'b0), .out(x92), .gate(not_4_out));
  Transistor #(.\type ("n")) transistor_507 (.in(1'b0), .out(x92), .gate(not_5_out));
  Pull_Resistor #(.pull(1)) pull_resistor_94 (.node(x93));
  Pull_Resistor #(.pull(1)) pull_resistor_95 (.node(x94));
  Transistor #(.\type ("n")) transistor_508 (.in(1'b0), .out(x93), .gate(n_T3));
  Transistor #(.\type ("n")) transistor_509 (.in(1'b0), .out(x93), .gate(or_1_out));
  Transistor #(.\type ("n")) transistor_510 (.in(1'b0), .out(x94), .gate(or_1_out));
  Transistor #(.\type ("n")) transistor_511 (.in(1'b0), .out(x94), .gate(IR7));
  Transistor #(.\type ("n")) transistor_512 (.in(1'b0), .out(x94), .gate(IR4));
  Transistor #(.\type ("n")) transistor_513 (.in(1'b0), .out(x93), .gate(not_4_out));
  Transistor #(.\type ("n")) transistor_514 (.in(1'b0), .out(x93), .gate(IR3));
  Transistor #(.\type ("n")) transistor_515 (.in(1'b0), .out(x94), .gate(IR3));
  Transistor #(.\type ("n")) transistor_516 (.in(1'b0), .out(x93), .gate(IR2));
  Transistor #(.\type ("n")) transistor_517 (.in(1'b0), .out(x94), .gate(IR2));
  Transistor #(.\type ("n")) transistor_518 (.in(1'b0), .out(x94), .gate(IR5));
  Pull_Resistor #(.pull(1)) pull_resistor_96 (.node(x95));
  Transistor #(.\type ("n")) transistor_519 (.in(1'b0), .out(x95), .gate(or_1_out));
  Transistor #(.\type ("n")) transistor_520 (.in(1'b0), .out(x95), .gate(IR7));
  Transistor #(.\type ("n")) transistor_521 (.in(1'b0), .out(x95), .gate(IR4));
  Transistor #(.\type ("n")) transistor_522 (.in(1'b0), .out(x95), .gate(IR3));
  Transistor #(.\type ("n")) transistor_523 (.in(1'b0), .out(x95), .gate(IR2));
  Transistor #(.\type ("n")) transistor_524 (.in(1'b0), .out(x95), .gate(IR6));
  Transistor #(.\type ("n")) transistor_525 (.in(1'b0), .out(x95), .gate(not_8_out));
  Pull_Resistor #(.pull(1)) pull_resistor_97 (.node(x96));
  Transistor #(.\type ("n")) transistor_526 (.in(1'b0), .out(x96), .gate(or_1_out));
  Transistor #(.\type ("n")) transistor_527 (.in(1'b0), .out(x96), .gate(IR7));
  Transistor #(.\type ("n")) transistor_528 (.in(1'b0), .out(x96), .gate(IR4));
  Transistor #(.\type ("n")) transistor_529 (.in(1'b0), .out(x96), .gate(not_5_out));
  Transistor #(.\type ("n")) transistor_530 (.in(1'b0), .out(x96), .gate(not_6_out));
  Transistor #(.\type ("n")) transistor_531 (.in(1'b0), .out(x96), .gate(not_7_out));
  Pull_Resistor #(.pull(1)) pull_resistor_98 (.node(x97));
  Transistor #(.\type ("n")) transistor_532 (.in(1'b0), .out(x97), .gate(not_3_out));
  Transistor #(.\type ("n")) transistor_533 (.in(1'b0), .out(x97), .gate(IR6));
  Transistor #(.\type ("n")) transistor_534 (.in(1'b0), .out(x97), .gate(IR5));
  Pull_Resistor #(.pull(1)) pull_resistor_99 (.node(x98));
  Transistor #(.\type ("n")) transistor_535 (.in(1'b0), .out(x98), .gate(n_T4));
  Transistor #(.\type ("n")) transistor_536 (.in(1'b0), .out(x98), .gate(or_1_out));
  Transistor #(.\type ("n")) transistor_537 (.in(1'b0), .out(x98), .gate(IR7));
  Transistor #(.\type ("n")) transistor_538 (.in(1'b0), .out(x98), .gate(IR4));
  Transistor #(.\type ("n")) transistor_539 (.in(1'b0), .out(x98), .gate(IR3));
  Transistor #(.\type ("n")) transistor_540 (.in(1'b0), .out(x98), .gate(IR2));
  Transistor #(.\type ("n")) transistor_541 (.in(1'b0), .out(x98), .gate(IR6));
  Transistor #(.\type ("n")) transistor_542 (.in(1'b0), .out(x98), .gate(IR5));
  Pull_Resistor #(.pull(1)) pull_resistor_100 (.node(x99));
  Pull_Resistor #(.pull(1)) pull_resistor_101 (.node(x100));
  Transistor #(.\type ("n")) transistor_543 (.in(1'b0), .out(x99), .gate(n_T2));
  Transistor #(.\type ("n")) transistor_544 (.in(1'b0), .out(x100), .gate(n_T2));
  Transistor #(.\type ("n")) transistor_545 (.in(1'b0), .out(x99), .gate(or_1_out));
  Transistor #(.\type ("n")) transistor_546 (.in(1'b0), .out(x100), .gate(or_1_out));
  Transistor #(.\type ("n")) transistor_547 (.in(1'b0), .out(x99), .gate(IR7));
  Transistor #(.\type ("n")) transistor_548 (.in(1'b0), .out(x100), .gate(IR7));
  Transistor #(.\type ("n")) transistor_549 (.in(1'b0), .out(x99), .gate(IR4));
  Transistor #(.\type ("n")) transistor_550 (.in(1'b0), .out(x100), .gate(IR4));
  Transistor #(.\type ("n")) transistor_551 (.in(1'b0), .out(x99), .gate(not_5_out));
  Transistor #(.\type ("n")) transistor_552 (.in(1'b0), .out(x100), .gate(not_5_out));
  Transistor #(.\type ("n")) transistor_553 (.in(1'b0), .out(x99), .gate(IR2));
  Transistor #(.\type ("n")) transistor_554 (.in(1'b0), .out(x100), .gate(IR2));
  Transistor #(.\type ("n")) transistor_555 (.in(1'b0), .out(x99), .gate(IR6));
  Transistor #(.\type ("n")) transistor_556 (.in(1'b0), .out(x99), .gate(IR5));
  Transistor #(.\type ("n")) transistor_557 (.in(1'b0), .out(x100), .gate(IR5));
  Pull_Resistor #(.pull(1)) pull_resistor_102 (.node(x101));
  Transistor #(.\type ("n")) transistor_558 (.in(1'b0), .out(x101), .gate(n_T4));
  Transistor #(.\type ("n")) transistor_559 (.in(1'b0), .out(x101), .gate(or_1_out));
  Transistor #(.\type ("n")) transistor_560 (.in(1'b0), .out(x101), .gate(IR7));
  Transistor #(.\type ("n")) transistor_561 (.in(1'b0), .out(x101), .gate(IR4));
  Transistor #(.\type ("n")) transistor_562 (.in(1'b0), .out(x101), .gate(not_5_out));
  Transistor #(.\type ("n")) transistor_563 (.in(1'b0), .out(x101), .gate(not_6_out));
  Transistor #(.\type ("n")) transistor_564 (.in(1'b0), .out(x101), .gate(not_7_out));
  Pull_Resistor #(.pull(1)) pull_resistor_103 (.node(x102));
  Transistor #(.\type ("n")) transistor_565 (.in(1'b0), .out(x102), .gate(n_T5));
  Transistor #(.\type ("n")) transistor_566 (.in(1'b0), .out(x102), .gate(or_1_out));
  Transistor #(.\type ("n")) transistor_567 (.in(1'b0), .out(x102), .gate(IR7));
  Transistor #(.\type ("n")) transistor_568 (.in(1'b0), .out(x102), .gate(IR4));
  Transistor #(.\type ("n")) transistor_569 (.in(1'b0), .out(x102), .gate(IR3));
  Transistor #(.\type ("n")) transistor_570 (.in(1'b0), .out(x102), .gate(IR2));
  Transistor #(.\type ("n")) transistor_571 (.in(1'b0), .out(x102), .gate(not_7_out));
  Pull_Resistor #(.pull(1)) pull_resistor_104 (.node(x103));
  Transistor #(.\type ("n")) transistor_572 (.in(1'b0), .out(x103), .gate(n_T5));
  Transistor #(.\type ("n")) transistor_573 (.in(1'b0), .out(x103), .gate(or_1_out));
  Transistor #(.\type ("n")) transistor_574 (.in(1'b0), .out(x103), .gate(IR7));
  Transistor #(.\type ("n")) transistor_575 (.in(1'b0), .out(x103), .gate(IR4));
  Transistor #(.\type ("n")) transistor_576 (.in(1'b0), .out(x103), .gate(IR3));
  Transistor #(.\type ("n")) transistor_577 (.in(1'b0), .out(x103), .gate(IR2));
  Transistor #(.\type ("n")) transistor_578 (.in(1'b0), .out(x103), .gate(IR6));
  Transistor #(.\type ("n")) transistor_579 (.in(1'b0), .out(x103), .gate(not_8_out));
  Pull_Resistor #(.pull(1)) pull_resistor_105 (.node(x104));
  Pull_Resistor #(.pull(1)) pull_resistor_106 (.node(x105));
  Transistor #(.\type ("n")) transistor_580 (.in(1'b0), .out(x105), .gate(n_T3));
  Transistor #(.\type ("n")) transistor_581 (.in(1'b0), .out(x104), .gate(n_T2));
  Transistor #(.\type ("n")) transistor_582 (.in(1'b0), .out(x104), .gate(or_1_out));
  Transistor #(.\type ("n")) transistor_583 (.in(1'b0), .out(x105), .gate(or_1_out));
  Transistor #(.\type ("n")) transistor_584 (.in(1'b0), .out(x104), .gate(IR7));
  Transistor #(.\type ("n")) transistor_585 (.in(1'b0), .out(x105), .gate(IR7));
  Transistor #(.\type ("n")) transistor_586 (.in(1'b0), .out(x104), .gate(IR4));
  Transistor #(.\type ("n")) transistor_587 (.in(1'b0), .out(x105), .gate(IR4));
  Transistor #(.\type ("n")) transistor_588 (.in(1'b0), .out(x104), .gate(not_5_out));
  Transistor #(.\type ("n")) transistor_589 (.in(1'b0), .out(x105), .gate(not_5_out));
  Transistor #(.\type ("n")) transistor_590 (.in(1'b0), .out(x105), .gate(IR2));
  Transistor #(.\type ("n")) transistor_591 (.in(1'b0), .out(x104), .gate(not_6_out));
  Transistor #(.\type ("n")) transistor_592 (.in(1'b0), .out(x104), .gate(not_7_out));
  Transistor #(.\type ("n")) transistor_593 (.in(1'b0), .out(x104), .gate(IR5));
  Transistor #(.\type ("n")) transistor_594 (.in(1'b0), .out(x105), .gate(not_8_out));
  Pull_Resistor #(.pull(1)) pull_resistor_107 (.node(x106));
  Transistor #(.\type ("n")) transistor_595 (.in(1'b0), .out(x106), .gate(not_1_out));
  Transistor #(.\type ("n")) transistor_596 (.in(1'b0), .out(x106), .gate(not_7_out));
  Pull_Resistor #(.pull(1)) pull_resistor_108 (.node(x107));
  Transistor #(.\type ("n")) transistor_597 (.in(1'b0), .out(x107), .gate(not_1_out));
  Transistor #(.\type ("n")) transistor_598 (.in(1'b0), .out(x107), .gate(IR7));
  Transistor #(.\type ("n")) transistor_599 (.in(1'b0), .out(x107), .gate(IR6));
  Pull_Resistor #(.pull(1)) pull_resistor_109 (.node(x108));
  Transistor #(.\type ("n")) transistor_600 (.in(1'b0), .out(x108), .gate(or_1_out));
  Transistor #(.\type ("n")) transistor_601 (.in(1'b0), .out(x108), .gate(IR7));
  Transistor #(.\type ("n")) transistor_602 (.in(1'b0), .out(x108), .gate(not_4_out));
  Transistor #(.\type ("n")) transistor_603 (.in(1'b0), .out(x108), .gate(not_5_out));
  Transistor #(.\type ("n")) transistor_604 (.in(1'b0), .out(x108), .gate(IR2));
  Transistor #(.\type ("n")) transistor_605 (.in(1'b0), .out(x108), .gate(not_7_out));
  Transistor #(.\type ("n")) transistor_606 (.in(1'b0), .out(x108), .gate(n_T0));
  Pull_Resistor #(.pull(1)) pull_resistor_110 (.node(x109));
  Transistor #(.\type ("n")) transistor_607 (.in(1'b0), .out(x109), .gate(or_1_out));
  Transistor #(.\type ("n")) transistor_608 (.in(1'b0), .out(x109), .gate(IR7));
  Transistor #(.\type ("n")) transistor_609 (.in(1'b0), .out(x109), .gate(IR4));
  Transistor #(.\type ("n")) transistor_610 (.in(1'b0), .out(x109), .gate(not_6_out));
  Transistor #(.\type ("n")) transistor_611 (.in(1'b0), .out(x109), .gate(IR6));
  Transistor #(.\type ("n")) transistor_612 (.in(1'b0), .out(x109), .gate(not_8_out));
  Transistor #(.\type ("n")) transistor_613 (.in(1'b0), .out(x109), .gate(n_T1X));
  Pull_Resistor #(.pull(1)) pull_resistor_111 (.node(x110));
  Pull_Resistor #(.pull(1)) pull_resistor_112 (.node(x111));
  Transistor #(.\type ("n")) transistor_614 (.in(1'b0), .out(x111), .gate(n_T3));
  Transistor #(.\type ("n")) transistor_615 (.in(1'b0), .out(x110), .gate(or_1_out));
  Transistor #(.\type ("n")) transistor_616 (.in(1'b0), .out(x110), .gate(IR7));
  Transistor #(.\type ("n")) transistor_617 (.in(1'b0), .out(x110), .gate(not_4_out));
  Transistor #(.\type ("n")) transistor_618 (.in(1'b0), .out(x111), .gate(not_4_out));
  Transistor #(.\type ("n")) transistor_619 (.in(1'b0), .out(x111), .gate(IR3));
  Transistor #(.\type ("n")) transistor_620 (.in(1'b0), .out(x110), .gate(not_5_out));
  Transistor #(.\type ("n")) transistor_621 (.in(1'b0), .out(x110), .gate(IR2));
  Transistor #(.\type ("n")) transistor_622 (.in(1'b0), .out(x111), .gate(not_6_out));
  Transistor #(.\type ("n")) transistor_623 (.in(1'b0), .out(x110), .gate(IR6));
  Transistor #(.\type ("n")) transistor_624 (.in(1'b0), .out(x110), .gate(n_T0));
  Pull_Resistor #(.pull(1)) pull_resistor_113 (.node(x112));
  Transistor #(.\type ("n")) transistor_625 (.in(1'b0), .out(x112), .gate(not_2_out));
  Transistor #(.\type ("n")) transistor_626 (.in(1'b0), .out(x112), .gate(not_7_out));
  Transistor #(.\type ("n")) transistor_627 (.in(1'b0), .out(x112), .gate(not_8_out));
  Transistor #(.\type ("n")) transistor_628 (.in(1'b0), .out(x112), .gate(n_T1X));
  Pull_Resistor #(.pull(1)) pull_resistor_114 (.node(x113));
  Transistor #(.\type ("n")) transistor_629 (.in(1'b0), .out(x113), .gate(or_1_out));
  Transistor #(.\type ("n")) transistor_630 (.in(1'b0), .out(x113), .gate(IR7));
  Transistor #(.\type ("n")) transistor_631 (.in(1'b0), .out(x113), .gate(IR4));
  Transistor #(.\type ("n")) transistor_632 (.in(1'b0), .out(x113), .gate(not_6_out));
  Transistor #(.\type ("n")) transistor_633 (.in(1'b0), .out(x113), .gate(IR6));
  Transistor #(.\type ("n")) transistor_634 (.in(1'b0), .out(x113), .gate(not_8_out));
  Transistor #(.\type ("n")) transistor_635 (.in(1'b0), .out(x113), .gate(n_T0));
  Pull_Resistor #(.pull(1)) pull_resistor_115 (.node(x114));
  Pull_Resistor #(.pull(1)) pull_resistor_116 (.node(x115));
  Transistor #(.\type ("n")) transistor_636 (.in(1'b0), .out(x115), .gate(n_T4));
  Transistor #(.\type ("n")) transistor_637 (.in(1'b0), .out(x114), .gate(or_1_out));
  Transistor #(.\type ("n")) transistor_638 (.in(1'b0), .out(x115), .gate(or_1_out));
  Transistor #(.\type ("n")) transistor_639 (.in(1'b0), .out(x114), .gate(IR7));
  Transistor #(.\type ("n")) transistor_640 (.in(1'b0), .out(x115), .gate(IR7));
  Transistor #(.\type ("n")) transistor_641 (.in(1'b0), .out(x114), .gate(IR4));
  Transistor #(.\type ("n")) transistor_642 (.in(1'b0), .out(x115), .gate(IR4));
  Transistor #(.\type ("n")) transistor_643 (.in(1'b0), .out(x115), .gate(IR3));
  Transistor #(.\type ("n")) transistor_644 (.in(1'b0), .out(x114), .gate(not_5_out));
  Transistor #(.\type ("n")) transistor_645 (.in(1'b0), .out(x114), .gate(IR2));
  Transistor #(.\type ("n")) transistor_646 (.in(1'b0), .out(x115), .gate(IR2));
  Transistor #(.\type ("n")) transistor_647 (.in(1'b0), .out(x114), .gate(IR6));
  Transistor #(.\type ("n")) transistor_648 (.in(1'b0), .out(x115), .gate(not_7_out));
  Transistor #(.\type ("n")) transistor_649 (.in(1'b0), .out(x115), .gate(IR5));
  Transistor #(.\type ("n")) transistor_650 (.in(1'b0), .out(x114), .gate(not_8_out));
  Transistor #(.\type ("n")) transistor_651 (.in(1'b0), .out(x114), .gate(n_T0));
  Pull_Resistor #(.pull(1)) pull_resistor_117 (.node(x116));
  Transistor #(.\type ("n")) transistor_652 (.in(1'b0), .out(x116), .gate(not_2_out));
  Transistor #(.\type ("n")) transistor_653 (.in(1'b0), .out(x116), .gate(not_3_out));
  Transistor #(.\type ("n")) transistor_654 (.in(1'b0), .out(x116), .gate(not_7_out));
  Transistor #(.\type ("n")) transistor_655 (.in(1'b0), .out(x116), .gate(IR5));
  Transistor #(.\type ("n")) transistor_656 (.in(1'b0), .out(x116), .gate(n_T1X));
  Pull_Resistor #(.pull(1)) pull_resistor_118 (.node(x117));
  Transistor #(.\type ("n")) transistor_657 (.in(1'b0), .out(x117), .gate(or_1_out));
  Transistor #(.\type ("n")) transistor_658 (.in(1'b0), .out(x117), .gate(not_3_out));
  Transistor #(.\type ("n")) transistor_659 (.in(1'b0), .out(x117), .gate(IR4));
  Transistor #(.\type ("n")) transistor_660 (.in(1'b0), .out(x117), .gate(not_5_out));
  Transistor #(.\type ("n")) transistor_661 (.in(1'b0), .out(x117), .gate(not_6_out));
  Transistor #(.\type ("n")) transistor_662 (.in(1'b0), .out(x117), .gate(not_7_out));
  Transistor #(.\type ("n")) transistor_663 (.in(1'b0), .out(x117), .gate(n_T1X));
  Pull_Resistor #(.pull(1)) pull_resistor_119 (.node(x118));
  Pull_Resistor #(.pull(1)) pull_resistor_120 (.node(x119));
  Transistor #(.\type ("n")) transistor_664 (.in(1'b0), .out(x118), .gate(not_1_out));
  Transistor #(.\type ("n")) transistor_665 (.in(1'b0), .out(x119), .gate(or_1_out));
  Transistor #(.\type ("n")) transistor_666 (.in(1'b0), .out(x118), .gate(IR7));
  Transistor #(.\type ("n")) transistor_667 (.in(1'b0), .out(x119), .gate(not_3_out));
  Transistor #(.\type ("n")) transistor_668 (.in(1'b0), .out(x118), .gate(IR4));
  Transistor #(.\type ("n")) transistor_669 (.in(1'b0), .out(x119), .gate(IR4));
  Transistor #(.\type ("n")) transistor_670 (.in(1'b0), .out(x119), .gate(IR3));
  Transistor #(.\type ("n")) transistor_671 (.in(1'b0), .out(x118), .gate(not_5_out));
  Transistor #(.\type ("n")) transistor_672 (.in(1'b0), .out(x118), .gate(IR2));
  Transistor #(.\type ("n")) transistor_673 (.in(1'b0), .out(x118), .gate(IR6));
  Transistor #(.\type ("n")) transistor_674 (.in(1'b0), .out(x119), .gate(not_7_out));
  Transistor #(.\type ("n")) transistor_675 (.in(1'b0), .out(x118), .gate(n_T1X));
  Transistor #(.\type ("n")) transistor_676 (.in(1'b0), .out(x119), .gate(n_T1X));
  Pull_Resistor #(.pull(1)) pull_resistor_121 (.node(x120));
  Pull_Resistor #(.pull(1)) pull_resistor_122 (.node(x121));
  Transistor #(.\type ("n")) transistor_677 (.in(1'b0), .out(x120), .gate(or_1_out));
  Transistor #(.\type ("n")) transistor_678 (.in(1'b0), .out(x120), .gate(not_3_out));
  Transistor #(.\type ("n")) transistor_679 (.in(1'b0), .out(x120), .gate(not_4_out));
  Transistor #(.\type ("n")) transistor_680 (.in(1'b0), .out(x120), .gate(not_5_out));
  Transistor #(.\type ("n")) transistor_681 (.in(1'b0), .out(x120), .gate(IR2));
  Transistor #(.\type ("n")) transistor_682 (.in(1'b0), .out(x121), .gate(IR6));
  Transistor #(.\type ("n")) transistor_683 (.in(1'b0), .out(x120), .gate(not_7_out));
  Transistor #(.\type ("n")) transistor_684 (.in(1'b0), .out(x120), .gate(n_T0));
  Pull_Resistor #(.pull(1)) pull_resistor_123 (.node(x122));
  Transistor #(.\type ("n")) transistor_685 (.in(1'b0), .out(x122), .gate(n_T3));
  Transistor #(.\type ("n")) transistor_686 (.in(1'b0), .out(x122), .gate(IR4));
  Transistor #(.\type ("n")) transistor_687 (.in(1'b0), .out(x122), .gate(not_5_out));
  Transistor #(.\type ("n")) transistor_688 (.in(1'b0), .out(x122), .gate(not_6_out));
  Pull_Resistor #(.pull(1)) pull_resistor_124 (.node(x123));
  Transistor #(.\type ("n")) transistor_689 (.in(1'b0), .out(x123), .gate(n_T2));
  Transistor #(.\type ("n")) transistor_690 (.in(1'b0), .out(x123), .gate(IR4));
  Transistor #(.\type ("n")) transistor_691 (.in(1'b0), .out(x123), .gate(IR3));
  Transistor #(.\type ("n")) transistor_692 (.in(1'b0), .out(x123), .gate(not_6_out));
  Pull_Resistor #(.pull(1)) pull_resistor_125 (.node(x124));
  Pull_Resistor #(.pull(1)) pull_resistor_126 (.node(x125));
  Transistor #(.\type ("n")) transistor_693 (.in(1'b0), .out(x124), .gate(n_T5));
  Transistor #(.\type ("n")) transistor_694 (.in(1'b0), .out(x125), .gate(n_T4));
  Transistor #(.\type ("n")) transistor_695 (.in(1'b0), .out(x124), .gate(not_2_out));
  Transistor #(.\type ("n")) transistor_696 (.in(1'b0), .out(x125), .gate(not_4_out));
  Transistor #(.\type ("n")) transistor_697 (.in(1'b0), .out(x124), .gate(IR3));
  Transistor #(.\type ("n")) transistor_698 (.in(1'b0), .out(x125), .gate(not_5_out));
  Transistor #(.\type ("n")) transistor_699 (.in(1'b0), .out(x124), .gate(IR2));
  Pull_Resistor #(.pull(1)) pull_resistor_127 (.node(x126));
  Transistor #(.\type ("n")) transistor_700 (.in(1'b0), .out(x126), .gate(IR7));
  Pull_Resistor #(.pull(1)) pull_resistor_128 (.node(x127));
  Transistor #(.\type ("n")) transistor_701 (.in(1'b0), .out(x127), .gate(or_1_out));
  Transistor #(.\type ("n")) transistor_702 (.in(1'b0), .out(x127), .gate(not_3_out));
  Transistor #(.\type ("n")) transistor_703 (.in(1'b0), .out(x127), .gate(not_4_out));
  Transistor #(.\type ("n")) transistor_704 (.in(1'b0), .out(x127), .gate(not_5_out));
  Transistor #(.\type ("n")) transistor_705 (.in(1'b0), .out(x127), .gate(IR2));
  Transistor #(.\type ("n")) transistor_706 (.in(1'b0), .out(x127), .gate(IR6));
  Transistor #(.\type ("n")) transistor_707 (.in(1'b0), .out(x127), .gate(not_8_out));
  Pull_Resistor #(.pull(1)) pull_resistor_129 (.node(x128));
  Pull_Resistor #(.pull(1)) pull_resistor_130 (.node(x129));
  Transistor #(.\type ("n")) transistor_708 (.in(1'b0), .out(x129), .gate(or_1_out));
  Transistor #(.\type ("n")) transistor_709 (.in(1'b0), .out(x129), .gate(IR7));
  Transistor #(.\type ("n")) transistor_710 (.in(1'b0), .out(x129), .gate(IR4));
  Transistor #(.\type ("n")) transistor_711 (.in(1'b0), .out(x128), .gate(not_5_out));
  Transistor #(.\type ("n")) transistor_712 (.in(1'b0), .out(x129), .gate(not_5_out));
  Transistor #(.\type ("n")) transistor_713 (.in(1'b0), .out(x128), .gate(IR2));
  Transistor #(.\type ("n")) transistor_714 (.in(1'b0), .out(x129), .gate(IR2));
endmodule

module PREDECODE (
  input  PHI2,
  input  Z_IR,
  input  D0,
  input  D1,
  input  D2,
  input  D3,
  input  D4,
  input  D5,
  input  D6,
  input  D7,
  output n_IMPLIED,
  output n_TWOCYCLE,
  output n_PD0,
  output n_PD1,
  output n_PD2,
  output n_PD3,
  output n_PD4,
  output n_PD5,
  output n_PD6,
  output n_PD7
);

  wire and_1_out, d_latch_1_not_q, d_latch_2_not_q, d_latch_3_not_q, d_latch_4_not_q, d_latch_5_not_q,
       d_latch_6_not_q, d_latch_7_not_q, d_latch_8_not_q, d_latch_9_q, d_latch_10_q, d_latch_11_q,
       d_latch_12_q, d_latch_13_q, d_latch_14_q, d_latch_15_q, d_latch_16_q, nor_1_out, nor_2_out, nor_3_out,
       nor_4_out, nor_5_out, nor_6_out, nor_7_out, nor_8_out, nor_9_out, nor_10_out, nor_11_out, nor_12_out,
       not_1_out;

  D_Latch d_latch_1 (.EN(1'b1), .D(D0), .NOT_Q(d_latch_1_not_q));  // open: Q
  D_Latch d_latch_2 (.EN(1'b1), .D(D1), .NOT_Q(d_latch_2_not_q));  // open: Q
  D_Latch d_latch_3 (.EN(1'b1), .D(D2), .NOT_Q(d_latch_3_not_q));  // open: Q
  D_Latch d_latch_4 (.EN(1'b1), .D(D3), .NOT_Q(d_latch_4_not_q));  // open: Q
  D_Latch d_latch_5 (.EN(1'b1), .D(D4), .NOT_Q(d_latch_5_not_q));  // open: Q
  D_Latch d_latch_6 (.EN(1'b1), .D(D5), .NOT_Q(d_latch_6_not_q));  // open: Q
  D_Latch d_latch_7 (.EN(1'b1), .D(D6), .NOT_Q(d_latch_7_not_q));  // open: Q
  D_Latch d_latch_8 (.EN(1'b1), .D(D7), .NOT_Q(d_latch_8_not_q));  // open: Q
  D_Latch d_latch_9 (.EN(PHI2), .D(d_latch_1_not_q), .Q(d_latch_9_q));  // open: NOT_Q
  D_Latch d_latch_10 (.EN(PHI2), .D(d_latch_2_not_q), .Q(d_latch_10_q));  // open: NOT_Q
  D_Latch d_latch_11 (.EN(PHI2), .D(d_latch_3_not_q), .Q(d_latch_11_q));  // open: NOT_Q
  D_Latch d_latch_12 (.EN(PHI2), .D(d_latch_4_not_q), .Q(d_latch_12_q));  // open: NOT_Q
  D_Latch d_latch_13 (.EN(PHI2), .D(d_latch_5_not_q), .Q(d_latch_13_q));  // open: NOT_Q
  D_Latch d_latch_14 (.EN(PHI2), .D(d_latch_6_not_q), .Q(d_latch_14_q));  // open: NOT_Q
  D_Latch d_latch_15 (.EN(PHI2), .D(d_latch_7_not_q), .Q(d_latch_15_q));  // open: NOT_Q
  D_Latch d_latch_16 (.EN(PHI2), .D(d_latch_8_not_q), .Q(d_latch_16_q));  // open: NOT_Q
  nor nor_1 (nor_1_out, d_latch_9_q, Z_IR);
  nor nor_2 (nor_2_out, d_latch_10_q, Z_IR);
  nor nor_3 (nor_3_out, d_latch_11_q, Z_IR);
  nor nor_4 (nor_4_out, d_latch_12_q, Z_IR);
  nor nor_5 (nor_5_out, d_latch_13_q, Z_IR);
  nor nor_6 (nor_6_out, d_latch_14_q, Z_IR);
  nor nor_7 (nor_7_out, d_latch_15_q, Z_IR);
  nor nor_8 (nor_8_out, d_latch_16_q, Z_IR);
  nor nor_9 (nor_9_out, nor_1_out, nor_3_out, n_PD3);
  nor nor_10 (nor_10_out, nor_2_out, nor_5_out, nor_8_out);
  not not_1 (not_1_out, nor_10_out);
  nor nor_11 (nor_11_out, n_PD0, nor_3_out, n_PD3, nor_5_out);
  nor nor_12 (nor_12_out, nor_1_out, nor_3_out, nor_4_out, nor_5_out, n_PD7);
  not not_2 (n_PD0, nor_1_out);
  not not_3 (n_PD1, nor_2_out);
  not not_4 (n_PD2, nor_3_out);
  not not_5 (n_PD3, nor_4_out);
  not not_6 (n_PD4, nor_5_out);
  not not_7 (n_PD5, nor_6_out);
  not not_8 (n_PD6, nor_7_out);
  not not_9 (n_PD7, nor_8_out);
  and and_1 (and_1_out, nor_9_out, not_1_out);
  not not_10 (n_IMPLIED, nor_9_out);
  nor nor_13 (n_TWOCYCLE, and_1_out, nor_11_out, nor_12_out);

  // Notes on the sheet:
  //   External databus
  //   transparent D-latches
  //   Keep D-latches
  //   0,2,~3
  //   1,4,7
  //   ~0,2,~3,4
  //   0,2,3,4,~7
endmodule
module RANDOM_LOGIC (
  input  PHI1,
  input  X0,
  input  X1,
  input  X2,
  input  X3,
  input  X4,
  input  X5,
  input  X6,
  input  X7,
  input  X8,
  input  X9,
  input  X10,
  input  X11,
  input  X12,
  input  X13,
  input  X14,
  input  X15,
  input  X16,
  input  X17,
  input  X18,
  input  X19,
  input  X20,
  input  X21,
  input  X22,
  input  X23,
  input  X24,
  input  X25,
  input  X26,
  input  X27,
  input  X28,
  input  X29,
  input  X30,
  input  X31,
  input  X32,
  input  X33,
  input  X34,
  input  X35,
  input  X36,
  input  X37,
  input  X38,
  input  X39,
  input  X40,
  input  X41,
  input  X42,
  input  X43,
  input  X44,
  input  X45,
  input  X46,
  input  X47,
  input  X48,
  input  X49,
  input  X50,
  input  X51,
  input  X52,
  input  X53,
  input  X54,
  input  X55,
  input  X56,
  input  X57,
  input  X58,
  input  X59,
  input  X60,
  input  X61,
  input  X62,
  input  X63,
  input  X64,
  input  X65,
  input  X66,
  input  X67,
  input  X68,
  input  X69,
  input  X70,
  input  X71,
  input  X72,
  input  X73,
  input  X74,
  input  X75,
  input  X76,
  input  X77,
  input  X78,
  input  X79,
  input  X80,
  input  X81,
  input  X82,
  input  X83,
  input  X84,
  input  X85,
  input  X86,
  input  X87,
  input  X88,
  input  X89,
  input  X90,
  input  X91,
  input  X92,
  input  X93,
  input  X94,
  input  X95,
  input  X96,
  input  X97,
  input  X98,
  input  X99,
  input  X100,
  input  X101,
  input  X102,
  input  X103,
  input  X104,
  input  X105,
  input  X106,
  input  X107,
  input  X108,
  input  X109,
  input  X110,
  input  X111,
  input  X112,
  input  X113,
  input  X114,
  input  X115,
  input  X116,
  input  X117,
  input  X118,
  input  X119,
  input  X120,
  input  X121,
  input  X122,
  input  X123,
  input  X124,
  input  X125,
  input  X126,
  input  X127,
  input  X128,
  input  X129,
  input  PHI2,
  input  IR0,
  input  n_IR5,
  input  n_NMIP,
  input  RESP,
  input  n_IRQP,
  input  AVR,
  input  ACR,
  input  SO,
  input  n_TWOCYCLE,
  input  n_IMPLIED,
  input  RDY,
  input  n_PRDY,
  input  DB7,
  input  DB6,
  input  DB5,
  input  DB4,
  input  DB3,
  input  DB2,
  input  DB1,
  input  DB0,
  output FETCH,
  output n_T0,
  output n_T2,
  output n_T3,
  output n_T4,
  output n_T5,
  output P_DB,
  output IR5_C,
  output Z_V,
  output DBZ_Z,
  output DB_P,
  output DB_V,
  output Z_ADL0,
  output Z_ADL2,
  output X_SB,
  output SB_X,
  output S_ADL,
  output S_S,
  output n_I_OUT,
  output n_C_OUT,
  output n_Z_OUT,
  output NDB_ADD,
  output Z_ADD,
  output ADL_ADD,
  output EORS,
  output n_ACIN,
  output n_DAA,
  output ADD_SB06,
  output n_DSA,
  output SRS,
  output DL_ADL,
  output DL_DB,
  output ADH_ABH,
  output SB_AC,
  output Z_ADH0,
  output AC_DB,
  output SB_ADH,
  output PCL_PCL,
  output PCL_ADL,
  output PCL_DB,
  output PCH_PCH,
  output Z_IR,
  output T1,
  output n_IPC,
  output IR5_I,
  output IR5_D,
  output ACR_C,
  output DB_N,
  output DB_C,
  output WR,
  output n_D_OUT,
  output n_N_OUT,
  output DB_ADD,
  output SB_ADD,
  output ANDS,
  output ORS,
  output SUMS,
  output PCH_ADH,
  output PCH_DB,
  output ADH_PCH,
  output n_T1X,
  output Z_ADL1,
  output Y_SB,
  output SB_Y,
  output S_SB,
  output SB_S,
  output n_V_OUT,
  output ADD_SB7,
  output ADD_ADL,
  output DL_ADH,
  output ADL_ABL,
  output AC_SB,
  output Z_ADH17,
  output SB_DB,
  output ADL_PCL,
  output DB_out7,
  output DB_out5,
  output DB_out3,
  output DB_out1,
  output DB_out6,
  output DB_out4,
  output DB_out2,
  output DB_out0
);

  wire alu_setup_1_and, alu_setup_1_inc_sb, alu_setup_1_sr, and_2_out, BR0, branch_logic_1_brfw,
       branch_logic_1_n_brtaken, BRK6E, bus_control_1_pgx, bus_control_1_ztst, dispatch_1_acrl2,
       dispatch_1_stor, dispatch_1_tres2, int_control_b_out, int_control_brk5_rdy, int_control_brk7,
       int_control_dores, int_control_n_donmi, n_ready, pc_setup_1_dl_pch, pc_setup_1_n_adl_pcl,
       pc_setup_1_n_pch_pch, pc_setup_1_pc_db, regs_control_1_n_sbxy, regs_control_1_stkop,
       regs_control_1_stxy, T0, T6, T7;

  INT_RESET_CONTROL int_control (
    .BR2(X80), .T0(T0), .BRK5(X22), .n_IRQP(n_IRQP), .n_I_OUT(n_I_OUT), .n_ready(n_ready), .PHI1(PHI1),
    .RESP(RESP), .PHI2(PHI2), .n_NMIP(n_NMIP), .B_OUT(int_control_b_out), .BRK6E(BRK6E),
    .BRK7(int_control_brk7), .BRK5_RDY(int_control_brk5_rdy), .DORES(int_control_dores),
    .n_DONMI(int_control_n_donmi));
  INT_VECTOR_Logic int_vector (
    .PHI2(PHI2), .BRK5_RDY(int_control_brk5_rdy), .BRK7(int_control_brk7), .DORES(int_control_dores),
    .n_DONMI(int_control_n_donmi), .Z_ADL0(Z_ADL0), .Z_ADL1(Z_ADL1), .Z_ADL2(Z_ADL2));
  REGS_CONTROL regs_control_1 (
    .STOR(dispatch_1_stor), .D35(X35), .D0(X0), .D1(X1), .D2(X2), .D3(X3), .D4(X4), .D5(X5), .D6(X6),
    .D7(X7), .D8(X8), .PHI1(PHI1), .D9(X9), .D10(X10), .D11(X11), .D12(X12), .D13(X13), .D14(X14), .D15(X15),
    .D16(X16), .D17(X17), .D18(X18), .PHI2(PHI2), .D19(X19), .D20(X20), .D21(X21), .D22(X22), .D23(X23),
    .D24(X24), .D25(X25), .D26(X26), .D48(X48), .n_ready(n_ready), .S_ADL(S_ADL), .Y_SB(Y_SB),
    .STXY(regs_control_1_stxy), .X_SB(X_SB), .S_SB(S_SB), .SB_X(SB_X), .n_SBXY(regs_control_1_n_sbxy),
    .SB_Y(SB_Y), .SB_S(SB_S), .S_S(S_S), .STKOP(regs_control_1_stkop));
  FLAGS flags_1 (
    .n_IR5(n_IR5), .DB0(DB0), .IR5_I(IR5_I), .BRK6E(BRK6E), .AVR(AVR), .DB_V(DB_V), .D112(X112), .Z_V(Z_V),
    .DB1(DB1), .SO(SO), .DB2(DB2), .DB3(DB3), .DB4(DB4), .P_DB(P_DB), .DB5(DB5), .DB6(DB6), .DB7(DB7),
    .DB_P(DB_P), .DBZ_Z(DBZ_Z), .DB_N(DB_N), .IR5_C(IR5_C), .ACR(ACR), .B_OUT(int_control_b_out),
    .DB_C(DB_C), .ACR_C(ACR_C), .IR5_D(IR5_D), .PHI1(PHI1), .PHI2(PHI2), .DB_out0(DB_out0),
    .DB_out1(DB_out1), .DB_out2(DB_out2), .DB_out3(DB_out3), .DB_out4(DB_out4), .DB_out5(DB_out5),
    .DB_out6(DB_out6), .DB_out7(DB_out7), .n_Z_OUT(n_Z_OUT), .n_N_OUT(n_N_OUT), .n_C_OUT(n_C_OUT),
    .n_D_OUT(n_D_OUT), .n_I_OUT(n_I_OUT), .n_V_OUT(n_V_OUT));
  ALU_SETUP alu_setup_1 (
    .D56(X56), .D69(X69), .D70(X70), .n_ready(n_ready), .D75(X75), .D76(X76), .D84(X84), .D85(X85),
    .D86(X86), .D87(X87), .D88(X88), .D89(X89), .T0(T0), .T1(T1), .BRK6E(BRK6E), .T6(T6), .T7(T7),
    .PGX(bus_control_1_pgx), .BR3(X93), .n_D_OUT(n_D_OUT), .n_C_OUT(n_C_OUT), .STKOP(regs_control_1_stkop),
    .PHI1(PHI1), .D26(X26), .D27(X27), .D29(X29), .D30(X30), .D31(X31), .D32(X32), .D33(X33), .D34(X34),
    .D35(X35), .D36(X36), .PHI2(PHI2), .D37(X37), .D38(X38), .D39(X39), .D40(X40), .D41(X41), .D42(X42),
    .D43(X43), .D44(X44), .D45(X45), .D47(X47), .BRFW(branch_logic_1_brfw), .D48(X48), .D49(X49), .D50(X50),
    .D51(X51), .D52(X52), .D53(X53), .D54(X54), .NDB_ADD(NDB_ADD), .ADD_SB06(ADD_SB06), .ADD_ADL(ADD_ADL),
    .n_DSA(n_DSA), .INC_SB(alu_setup_1_inc_sb), .SR(alu_setup_1_sr), .DB_ADD(DB_ADD), .Z_ADD(Z_ADD),
    .SB_ADD(SB_ADD), .ADL_ADD(ADL_ADD), .AND(alu_setup_1_and), .ANDS(ANDS), .EORS(EORS), .ORS(ORS),
    .n_ACIN(n_ACIN), .SRS(SRS), .SUMS(SUMS), .n_DAA(n_DAA), .ADD_SB7(ADD_SB7));
  and and_1 (BR0, X73, ~n_PRDY);  // AND_Gate
  BUS_CONTROL bus_control_1 (
    .D129(X129), .Z_ADL0(Z_ADL0), .BR2(X80), .ACRL2(dispatch_1_acrl2), .D55(X55), .DL_PCH(pc_setup_1_dl_pch),
    .BR3(X93), .n_ready(n_ready), .T2(X28), .INC_SB(alu_setup_1_inc_sb), .D45(X45), .BRK6E(BRK6E), .D46(X46),
    .D47(X47), .D48(X48), .D57(X57), .STXY(regs_control_1_stxy), .D101(X101),
    .n_PCH_PCH(pc_setup_1_n_pch_pch), .T0(T0), .T1(T1), .T6(T6), .T7(T7), .D56(X56), .D58(X58), .PHI1(PHI1),
    .D59(X59), .D60(X60), .D61(X61), .D62(X62), .D63(X63), .D64(X64), .D65(X65), .D66(X66), .D67(X67),
    .D68(X68), .PHI2(PHI2), .AND(alu_setup_1_and), .D71(X71), .D72(X72), .D73(BR0), .D74(X74), .D79(X79),
    .STOR(dispatch_1_stor), .D81(X81), .D82(X82), .D84(X84), .n_SBXY(regs_control_1_n_sbxy), .D89(X89),
    .D90(X90), .D91(X91), .D83(X83), .D128(and_2_out), .Z_ADH0(Z_ADH0), .ADH_ABH(ADH_ABH), .DL_DB(DL_DB),
    .Z_ADH17(Z_ADH17), .SB_AC(SB_AC), .ZTST(bus_control_1_ztst), .ADL_ABL(ADL_ABL), .AC_SB(AC_SB),
    .SB_DB(SB_DB), .AC_DB(AC_DB), .PGX(bus_control_1_pgx), .SB_ADH(SB_ADH), .DL_ADH(DL_ADH), .DL_ADL(DL_ADL));
  PC_SETUP pc_setup_1 (
    .D56(X56), .D77(X77), .D78(X78), .D83(X83), .D84(X84), .D94(X94), .D95(X95), .D96(X96), .PHI1(PHI1),
    .D129(X129), .n_ready(n_ready), .BR3(X93), .BR2(X80), .T0(T0), .T1(T1), .BR0(BR0), .PHI2(PHI2),
    .PCL_DB(PCL_DB), .PCH_DB(PCH_DB), .PC_DB(pc_setup_1_pc_db), .PCL_ADL(PCL_ADL), .PCH_ADH(PCH_ADH),
    .PCL_PCL(PCL_PCL), .ADL_PCL(ADL_PCL), .n_ADL_PCL(pc_setup_1_n_adl_pcl), .DL_PCH(pc_setup_1_dl_pch),
    .ADH_PCH(ADH_PCH), .PCH_PCH(PCH_PCH), .n_PCH_PCH(pc_setup_1_n_pch_pch));
  DISPATCH dispatch_1 (
    .n_BRTAKEN(branch_logic_1_n_brtaken), .n_TWOCYCLE(n_TWOCYCLE), .n_ADL_PCL(pc_setup_1_n_adl_pcl),
    .BRK6E(BRK6E), .n_IMPLIED(n_IMPLIED), .BR2(X80), .RESP(RESP), .ACR(ACR), .DORES(int_control_dores),
    .PC_DB(pc_setup_1_pc_db), .D91(X91), .D92(X92), .BR3(X93), .D96(X96), .D97(X97), .PHI1(PHI1), .D98(X98),
    .D100(X100), .D101(X101), .D102(X102), .D103(X103), .D104(X104), .D105(X105), .D106(X106), .D107(X107),
    .D111(X111), .PHI2(PHI2), .D122(X122), .D123(X123), .D124(X124), .D125(X125), .RDY(RDY),
    .B_OUT(int_control_b_out), .BRFW(branch_logic_1_brfw), .WR(WR), .T1(T1), .n_T0(n_T0), .T0(T0),
    .n_T1X(n_T1X), .T6(T6), .n_IPC(n_IPC), .T7(T7), .ACRL2(dispatch_1_acrl2), .TRES2(dispatch_1_tres2),
    .STOR(dispatch_1_stor), .Z_IR(Z_IR), .FETCH(FETCH), .n_ready(n_ready));
  FLAGS_CONTROL flags_control_1 (
    .D99(X99), .D108(X108), .D110(X110), .D120(X120), .D127(X127), .D107(X107), .PHI2(PHI2), .T7(T7),
    .D112(X112), .D116(X116), .D117(X117), .D118(X118), .D119(X119), .ZTST(bus_control_1_ztst), .D109(X109),
    .n_ready(n_ready), .SR(alu_setup_1_sr), .D114(X114), .D115(X115), .D98(X98), .D113(X113), .IR5_I(IR5_I),
    .IR5_C(IR5_C), .IR5_D(IR5_D), .Z_V(Z_V), .ACR_C(ACR_C), .DBZ_Z(DBZ_Z), .P_DB(P_DB), .DB_N(DB_N),
    .DB_P(DB_P), .DB_C(DB_C), .DB_V(DB_V));
  and and_2 (and_2_out, X128, ~IR0);  // AND_Gate
  BRANCH_LOGIC branch_logic_1 (
    .D126(X126), .n_C_OUT(n_C_OUT), .n_V_OUT(n_V_OUT), .n_N_OUT(n_N_OUT), .n_IR5(n_IR5), .n_Z_OUT(n_Z_OUT),
    .PHI1(PHI1), .PHI2(PHI2), .DB7_in(DB7), .BR2(X80), .D121(X121), .n_BRTAKEN(branch_logic_1_n_brtaken),
    .BRFW(branch_logic_1_brfw));
  EXTENDED_CYCLE_COUNTER extended_cycle_counter_1 (
    .TRES2(dispatch_1_tres2), .n_ready(n_ready), .T1(T1), .PHI1(PHI1), .PHI2(PHI2), .n_T2(n_T2), .n_T3(n_T3),
    .n_T4(n_T4), .n_T5(n_T5));

  // Other names for the same wires on the sheet: BR2 = X80; BR3 = X93; T2 = X28

  // Notes on the sheet:
  //   BRK5
  //   JSR2
  //   STK2
  //   Branch T0 Skip
  //   Push/pull
endmodule

module NMI_FF (
  input  n_NMI,
  input  PHI2,
  output NMIP
);

  wire and_1_out, and_2_out, nor_1_out, nor_2_out, not_1_out;

  not not_1 (not_1_out, n_NMI);
  and and_1 (and_1_out, not_1_out, PHI2);
  nor nor_1 (nor_1_out, and_2_out, nor_2_out);
  and and_2 (and_2_out, n_NMI, PHI2);
  nor nor_2 (nor_2_out, nor_1_out, and_1_out);
  not not_2 (NMIP, nor_2_out);
endmodule

module INT_RESET_CONTROL (
  input  PHI1,
  input  PHI2,
  input  BRK5,
  input  n_ready,
  input  RESP,
  input  n_NMIP,
  input  BR2,
  input  T0,
  input  n_IRQP,
  input  n_I_OUT,
  output BRK6E,
  output BRK7,
  output BRK5_RDY,
  output DORES,
  output n_DONMI,
  output B_OUT
);

  wire and_2_out, and_3_out, b_latch1_q, b_latch2_q, brk5_latch_q, brk6_latch1_not_q, brk6_latch2_not_q,
       brk6e_latch_q, brk7_latch_not_q, delay_latch1_not_q, delay_latch2_q, donmi_latch_q, ff1_latch_q,
       ff2_latch_q, nand_1_out, nand_2_out, nand_3_out, nmip_latch_q, nor_1_out, nor_2_out, nor_3_out,
       nor_4_out, nor_5_out, nor_6_out, nor_9_out, not_1_out, not_2_out, not_3_out, not_4_out, or_1_out,
       or_2_out, res_latch1_q, res_latch2_q;

  and and_1 (BRK5_RDY, BRK5, not_1_out);
  not not_1 (not_1_out, n_ready);
  not not_2 (not_2_out, brk5_latch_q);
  D_Latch brk5_latch (.EN(PHI2), .D(BRK5_RDY), .Q(brk5_latch_q));  // open: NOT_Q
  D_Latch res_latch1 (.EN(PHI2), .D(RESP), .Q(res_latch1_q));  // open: NOT_Q
  D_Latch res_latch2 (.EN(PHI1), .D(nor_4_out), .Q(res_latch2_q));  // open: NOT_Q
  D_Latch brk7_latch (.EN(PHI2), .D(BRK7), .NOT_Q(brk7_latch_not_q));  // open: Q
  D_Latch nmip_latch (.EN(PHI1), .D(n_NMIP), .Q(nmip_latch_q));  // open: NOT_Q
  D_Latch delay_latch1 (.EN(PHI2), .D(n_DONMI), .NOT_Q(delay_latch1_not_q));  // open: Q
  D_Latch ff1_latch (.EN(PHI2), .D(n_DONMI), .Q(ff1_latch_q));  // open: NOT_Q
  D_Latch brk6e_latch (.EN(PHI1), .D(BRK6E), .Q(brk6e_latch_q));  // open: NOT_Q
  or or_1 (or_1_out, n_IRQP, not_3_out);
  not not_3 (not_3_out, n_I_OUT);
  D_Latch b_latch2 (.EN(PHI1), .D(nor_9_out), .Q(b_latch2_q));  // open: NOT_Q
  not not_4 (not_4_out, b_latch2_q);
  and and_2 (and_2_out, not_2_out, nand_1_out);
  nand nand_1 (nand_1_out, n_ready, brk6_latch1_not_q);
  nor nor_1 (nor_1_out, res_latch1_q, res_latch2_q);
  nor nor_2 (nor_2_out, nmip_latch_q, nor_6_out);
  D_Latch ff2_latch (.EN(PHI2), .D(nor_2_out), .Q(ff2_latch_q));  // open: NOT_Q
  D_Latch delay_latch2 (.EN(PHI1), .D(delay_latch1_not_q), .Q(delay_latch2_q));  // open: NOT_Q
  nor nor_3 (nor_3_out, ff1_latch_q, brk6e_latch_q);
  nand nand_2 (nand_2_out, or_1_out, n_DONMI);
  and and_3 (and_3_out, nand_3_out, not_4_out);
  D_Latch brk6_latch1 (.EN(PHI1), .D(and_2_out), .NOT_Q(brk6_latch1_not_q));  // open: Q
  nor nor_4 (nor_4_out, nor_1_out, BRK6E);
  nor nor_5 (nor_5_out, brk7_latch_not_q, n_NMIP, nor_2_out);
  nor nor_6 (nor_6_out, ff2_latch_q, delay_latch2_q);
  nor nor_7 (n_DONMI, donmi_latch_q, nor_3_out);
  or or_2 (or_2_out, BR2, T0);
  D_Latch b_latch1 (.EN(PHI2), .D(and_3_out), .Q(b_latch1_q));  // open: NOT_Q
  D_Latch brk6_latch2 (.EN(PHI2), .D(brk6_latch1_not_q), .NOT_Q(brk6_latch2_not_q));  // open: Q
  nor nor_8 (BRK7, brk6_latch1_not_q, BRK5_RDY);
  not not_5 (DORES, nor_1_out);
  D_Latch donmi_latch (.EN(PHI1), .D(nor_5_out), .Q(donmi_latch_q));  // open: NOT_Q
  nand nand_3 (nand_3_out, or_2_out, nand_2_out);
  nor nor_9 (nor_9_out, b_latch1_q, BRK6E);
  nor nor_10 (BRK6E, brk6_latch2_not_q, n_ready);
  nor nor_11 (B_OUT, DORES, nor_9_out);

  // Notes on the sheet:
  //   /NMIP
  //   /IRQP
  //   INTERRUPT CYCLE 6-7
  //   BRK_FF
  //   RESET FLIP/FLOP
  //   RES_FF
  //   NMI EDGE DETECT
  //   NMI_FF1
  //   INTERRUPT CHECK
  //   BR2
  //   T0
  //   B FLAG
  //   B_FF
  //   NMI_FF2
  //   /DONMI
  //   /DONMI
endmodule

module INT_VECTOR_Logic (
  input  PHI2,
  input  BRK5_RDY,
  input  BRK7,
  input  DORES,
  input  n_DONMI,
  output Z_ADL0,
  output Z_ADL1,
  output Z_ADL2
);

  wire nor_1_out, nor_2_out, not_1_out, not_2_out, not_3_out, zadl2_latch_not_q;

  not not_1 (not_1_out, DORES);
  not not_2 (not_2_out, BRK5_RDY);
  nor nor_1 (nor_1_out, BRK7, not_1_out);
  nor nor_2 (nor_2_out, BRK7, DORES, n_DONMI);
  not not_3 (not_3_out, nor_1_out);
  D_Latch zadl0_latch (.EN(PHI2), .D(not_2_out), .NOT_Q(Z_ADL0));  // open: Q
  D_Latch zadl1_latch (.EN(PHI2), .D(not_3_out), .NOT_Q(Z_ADL1));  // open: Q
  D_Latch zadl2_latch (.EN(PHI2), .D(nor_2_out), .NOT_Q(zadl2_latch_not_q));  // open: Q
  not not_4 (Z_ADL2, zadl2_latch_not_q);

  // Notes on the sheet:
  //   FFFA:NMI, 1010
  //   FFFC:RESET, 1100
  //   FFFE:IRQ/BRK, 1110
endmodule

module REGS_CONTROL (
  input  PHI1,
  input  PHI2,
  input  STOR,
  input  D0,
  input  D1,
  input  D2,
  input  D3,
  input  D4,
  input  D5,
  input  D6,
  input  D7,
  input  D8,
  input  D9,
  input  D10,
  input  D11,
  input  D12,
  input  D13,
  input  D14,
  input  D15,
  input  D16,
  input  D17,
  input  D18,
  input  D19,
  input  D20,
  input  D21,
  input  D22,
  input  D23,
  input  D24,
  input  D25,
  input  D26,
  input  D48,
  input  n_ready,
  input  D35,
  output Y_SB,
  output STXY,
  output X_SB,
  output S_SB,
  output SB_X,
  output n_SBXY,
  output SB_Y,
  output SB_S,
  output S_S,
  output STKOP,
  output S_ADL
);

  wire and_1_out, and_2_out, and_3_out, and_4_out, and_5_out, and_6_out, and_7_out, nor_1_out, nor_2_out,
       nor_3_out, nor_4_out, nor_5_out, nor_6_out, nor_8_out, nor_9_out, nor_11_out, nor_12_out, nor_13_out,
       nor_14_out, nor_15_out, nor_16_out, not_1_out, not_2_out, not_3_out, not_4_out, nready_latch_not_q,
       nready_latch_q, sadl_latch_not_q, sbs_latch_q, sbx_latch_q, sby_latch_q, ss_latch_q, ssb_latch_not_q,
       xsb_latch_q, ysb_latch_q;

  and and_1 (and_1_out, D6, D7);
  and and_2 (and_2_out, D6, not_1_out);
  not not_1 (not_1_out, D7);
  nor nor_1 (nor_1_out, D14, D15, D16);
  not not_2 (not_2_out, D17);
  nor nor_2 (nor_2_out, D18, D19, D20);
  not not_3 (not_3_out, D48);
  nor nor_3 (nor_3_out, D21, D22, D23, D24, D25, D26);
  and and_3 (and_3_out, STOR, D0);
  and and_4 (and_4_out, STOR, D12);
  D_Latch nready_latch (.EN(PHI1), .D(n_ready), .Q(nready_latch_q), .NOT_Q(nready_latch_not_q));
  nor nor_4 (nor_4_out, not_3_out, n_ready);
  nor nor_5 (nor_5_out, D1, D2, D3, D4, D5, and_1_out, and_3_out);
  nor nor_6 (nor_6_out, and_4_out, and_2_out, D8, D9, D10, D11, D13);
  and and_5 (and_5_out, D21, nready_latch_not_q);
  nor nor_7 (STKOP, nor_3_out, nready_latch_q);
  and and_6 (and_6_out, STOR, D0);
  and and_7 (and_7_out, STOR, D12);
  nand nand_1 (n_SBXY, nor_1_out, nor_2_out);
  nor nor_8 (nor_8_out, D13, nor_4_out, STKOP);
  nor nor_9 (nor_9_out, and_5_out, D35);
  not not_4 (not_4_out, nor_8_out);
  D_Latch ysb_latch (.EN(PHI2), .D(nor_5_out), .Q(ysb_latch_q));  // open: NOT_Q
  nor nor_10 (STXY, and_6_out, and_7_out);
  D_Latch xsb_latch (.EN(PHI2), .D(nor_6_out), .Q(xsb_latch_q));  // open: NOT_Q
  D_Latch ssb_latch (.EN(PHI2), .D(not_2_out), .NOT_Q(ssb_latch_not_q));  // open: Q
  D_Latch sbx_latch (.EN(PHI2), .D(nor_1_out), .Q(sbx_latch_q));  // open: NOT_Q
  D_Latch sby_latch (.EN(PHI2), .D(nor_2_out), .Q(sby_latch_q));  // open: NOT_Q
  D_Latch sbs_latch (.EN(PHI2), .D(nor_8_out), .Q(sbs_latch_q));  // open: NOT_Q
  D_Latch ss_latch (.EN(PHI2), .D(not_4_out), .Q(ss_latch_q));  // open: NOT_Q
  D_Latch sadl_latch (.EN(PHI2), .D(nor_9_out), .NOT_Q(sadl_latch_not_q));  // open: Q
  nor nor_11 (nor_11_out, ysb_latch_q, PHI2);
  buf buffer_1 (Y_SB, nor_11_out);
  nor nor_12 (nor_12_out, xsb_latch_q, PHI2);
  buf buffer_2 (X_SB, nor_12_out);
  buf buffer_3 (S_SB, ssb_latch_not_q);
  nor nor_13 (nor_13_out, sbx_latch_q, PHI2);
  buf buffer_4 (SB_X, nor_13_out);
  nor nor_14 (nor_14_out, sby_latch_q, PHI2);
  buf buffer_5 (SB_Y, nor_14_out);
  nor nor_15 (nor_15_out, sbs_latch_q, PHI2);
  buf buffer_6 (SB_S, nor_15_out);
  nor nor_16 (nor_16_out, ss_latch_q, PHI2);
  buf buffer_7 (S_S, nor_16_out);
  buf buffer_8 (S_ADL, sadl_latch_not_q);

  // Notes on the sheet:
  //   JSR2
  //   STK2
  //   TXS
  //   #SB/X
  //   #S/SB
  //   #SB/Y
  //   STOR
  //   STOR
  //   STKOP
  //   #Y/SB
  //   #X/SB
  //   #S/SB
  //   #SBXY
  //   #SB/S
  //   #S/ADL
endmodule

module EXTENDED_CYCLE_COUNTER (
  input  PHI1,
  input  PHI2,
  input  TRES2,
  input  n_ready,
  input  T1,
  output n_T2,
  output n_T3,
  output n_T4,
  output n_T5
);

  wire multiplexer_1_out, multiplexer_2_out, multiplexer_3_out, multiplexer_4_out, nor_1_out, nor_2_out,
       nor_3_out, nor_4_out, t1_latch_not_q, t2_latch1_q, t2_latch2_not_q, t3_latch1_q, t3_latch2_not_q,
       t4_latch1_q, t4_latch2_not_q, t5_latch1_q, t5_latch2_not_q;

  D_Latch t1_latch (.EN(PHI2), .D(T1), .NOT_Q(t1_latch_not_q));  // open: Q
  Multiplexer multiplexer_1 (.in0(t1_latch_not_q), .in1(t2_latch2_not_q), .out(multiplexer_1_out), .sel(n_ready));
  Multiplexer multiplexer_2 (.in0(t2_latch2_not_q), .in1(t3_latch2_not_q), .out(multiplexer_2_out), .sel(n_ready));
  Multiplexer multiplexer_3 (.in0(t3_latch2_not_q), .in1(t4_latch2_not_q), .out(multiplexer_3_out), .sel(n_ready));
  Multiplexer multiplexer_4 (.in0(t4_latch2_not_q), .in1(t5_latch2_not_q), .out(multiplexer_4_out), .sel(n_ready));
  nor nor_1 (nor_1_out, TRES2, t2_latch1_q);
  nor nor_2 (nor_2_out, TRES2, t3_latch1_q);
  nor nor_3 (nor_3_out, TRES2, t4_latch1_q);
  nor nor_4 (nor_4_out, TRES2, t5_latch1_q);
  D_Latch t2_latch2 (.EN(PHI2), .D(nor_1_out), .NOT_Q(t2_latch2_not_q));  // open: Q
  D_Latch t2_latch1 (.EN(PHI1), .D(multiplexer_1_out), .Q(t2_latch1_q));  // open: NOT_Q
  D_Latch t3_latch2 (.EN(PHI2), .D(nor_2_out), .NOT_Q(t3_latch2_not_q));  // open: Q
  D_Latch t3_latch1 (.EN(PHI1), .D(multiplexer_2_out), .Q(t3_latch1_q));  // open: NOT_Q
  D_Latch t4_latch2 (.EN(PHI2), .D(nor_3_out), .NOT_Q(t4_latch2_not_q));  // open: Q
  D_Latch t4_latch1 (.EN(PHI1), .D(multiplexer_3_out), .Q(t4_latch1_q));  // open: NOT_Q
  D_Latch t5_latch2 (.EN(PHI2), .D(nor_4_out), .NOT_Q(t5_latch2_not_q));  // open: Q
  D_Latch t5_latch1 (.EN(PHI1), .D(multiplexer_4_out), .Q(t5_latch1_q));  // open: NOT_Q
  not not_1 (n_T2, nor_1_out);
  not not_2 (n_T3, nor_2_out);
  not not_3 (n_T4, nor_3_out);
  not not_4 (n_T5, nor_4_out);
endmodule

module ALU_SETUP (
  input  PHI1,
  input  PHI2,
  input  BRFW,
  input  n_ready,
  input  BRK6E,
  input  STKOP,
  input  D26,
  input  D27,
  input  D29,
  input  D30,
  input  D31,
  input  D32,
  input  D33,
  input  D34,
  input  D35,
  input  D36,
  input  D37,
  input  D38,
  input  D39,
  input  D40,
  input  D41,
  input  D42,
  input  D43,
  input  D44,
  input  D45,
  input  D47,
  input  D48,
  input  D49,
  input  D50,
  input  D51,
  input  D52,
  input  D53,
  input  D54,
  input  D56,
  input  D69,
  input  D70,
  input  D75,
  input  D76,
  input  D84,
  input  D85,
  input  D86,
  input  D87,
  input  D88,
  input  D89,
  input  T0,
  input  T1,
  input  T6,
  input  T7,
  input  PGX,
  input  BR3,
  input  n_D_OUT,
  input  n_C_OUT,
  output NDB_ADD,
  output DB_ADD,
  output Z_ADD,
  output SB_ADD,
  output ADL_ADD,
  output AND,
  output ANDS,
  output EORS,
  output ORS,
  output n_ACIN,
  output SRS,
  output SUMS,
  output n_DAA,
  output ADD_SB7,
  output ADD_SB06,
  output ADD_ADL,
  output n_DSA,
  output INC_SB,
  output SR
);

  wire acin_latch1_q, acin_latch2_q, acin_latch3_q, acin_latch4_q, acin_latch5_not_q, add_sb7_inst_n_add_sb7,
       addadl_latch_not_q, addsb06_latch_not_q, addsb7_latch_q, adladd_latch_q, and_1_out, and_2_out,
       and_3_out, ands_latch1_not_q, ands_latch2_not_q, daa_latch1_not_q, daa_latch2_not_q, dbadd_latch_q,
       dsa_latch1_not_q, eors_latch1_not_q, eors_latch2_not_q, nand_1_out, nand_2_out, nand_3_out,
       nand_4_out, nand_5_out, nand_6_out, ndbadd_latch_q, nor_1_out, nor_2_out, nor_3_out, nor_4_out,
       nor_5_out, nor_6_out, nor_7_out, nor_8_out, nor_9_out, nor_10_out, nor_11_out, nor_12_out, nor_13_out,
       nor_14_out, nor_15_out, nor_16_out, nor_17_out, nor_18_out, nor_19_out, nor_20_out, nor_21_out,
       nor_22_out, nor_23_out, not_1_out, not_2_out, not_4_out, not_5_out, not_6_out, not_9_out, not_10_out,
       not_11_out, not_12_out, not_13_out, not_14_out, not_15_out, or_1_out, or_2_out, ors_latch1_not_q,
       ors_latch2_not_q, sbadd_latch_q, srs_latch1_not_q, srs_latch2_not_q, sums_latch1_not_q,
       sums_latch2_not_q, zadd_latch_q;

  not not_1 (not_1_out, D34);
  not not_2 (not_2_out, n_D_OUT);
  nor nor_1 (nor_1_out, D32, n_ready);
  and and_1 (and_1_out, D33, not_1_out);
  and and_2 (and_2_out, T6, D44);
  or or_1 (or_1_out, D52, D53);
  nor nor_2 (nor_2_out, D69, D70);
  not not_3 (AND, nor_2_out);
  and and_3 (and_3_out, D76, T6);
  not not_4 (not_4_out, D27);
  not not_5 (not_5_out, nor_1_out);
  nor nor_3 (nor_3_out, and_1_out, D35, D36, D37, D38, D39, n_ready);
  nor nor_4 (nor_4_out, D39, D40, D41, D42, D43, and_2_out);
  not not_6 (not_6_out, BR3);
  nor nor_5 (nor_5_out, D75, and_3_out);
  not not_7 (SR, nor_5_out);
  nor nor_6 (nor_6_out, D84, D85, D86, D87, D88, D89, D26);
  not not_8 (INC_SB, nor_4_out);
  nor nor_7 (nor_7_out, not_6_out, BRFW);
  nor nor_8 (nor_8_out, T0, T6);
  not not_9 (not_9_out, D47);
  nor nor_9 (nor_9_out, D49, D50, nor_7_out);
  not not_10 (not_10_out, nor_9_out);
  nor nor_10 (nor_10_out, n_C_OUT, nor_8_out);
  nor nor_11 (nor_11_out, STKOP, D30, D31, D45, D48, INC_SB, D47, BRK6E, n_ready);
  nor nor_12 (nor_12_out, nor_3_out, not_9_out);
  nand nand_1 (nand_1_out, nor_10_out, or_1_out);
  not not_11 (not_11_out, D54);
  nand nand_2 (nand_2_out, nand_1_out, not_11_out);
  nand nand_3 (nand_3_out, D52, not_2_out);
  nor nor_13 (nor_13_out, nor_6_out, PGX);
  nor nor_14 (nor_14_out, nand_3_out, D51);
  nand nand_4 (nand_4_out, D51, not_2_out);
  or or_2 (or_2_out, not_10_out, D56, D51);
  D_Latch acin_latch1 (.EN(PHI2), .D(nor_12_out), .Q(acin_latch1_q));  // open: NOT_Q
  D_Latch acin_latch2 (.EN(PHI2), .D(INC_SB), .Q(acin_latch2_q));  // open: NOT_Q
  D_Latch acin_latch3 (.EN(PHI2), .D(not_10_out), .Q(acin_latch3_q));  // open: NOT_Q
  D_Latch acin_latch4 (.EN(PHI2), .D(nand_2_out), .Q(acin_latch4_q));  // open: NOT_Q
  not not_12 (not_12_out, nor_13_out);
  not not_13 (not_13_out, nor_14_out);
  not not_14 (not_14_out, n_ready);
  nor nor_15 (nor_15_out, acin_latch1_q, acin_latch2_q, acin_latch3_q, acin_latch4_q);
  nand nand_5 (nand_5_out, or_2_out, not_14_out);
  ADD_SB7_Logic add_sb7_inst (
    .n_C_OUT(n_C_OUT), .n_ready(n_ready), .SR(SR), .n_ROR(not_4_out), .PHI1(PHI1), .PHI2(PHI2),
    .n_ADD_SB7(add_sb7_inst_n_add_sb7));
  nor nor_16 (nor_16_out, T7, STKOP, D56, T1, PGX);
  nand nand_6 (nand_6_out, nand_5_out, nor_3_out);
  nor nor_17 (nor_17_out, AND, D29, not_5_out, SR);
  nor nor_18 (nor_18_out, nor_16_out, add_sb7_inst_n_add_sb7);
  not not_15 (not_15_out, nor_11_out);
  D_Latch ndbadd_latch (.EN(PHI2), .D(nand_5_out), .Q(ndbadd_latch_q));  // open: NOT_Q
  D_Latch dbadd_latch (.EN(PHI2), .D(nand_6_out), .Q(dbadd_latch_q));  // open: NOT_Q
  D_Latch zadd_latch (.EN(PHI2), .D(nor_11_out), .Q(zadd_latch_q));  // open: NOT_Q
  D_Latch sbadd_latch (.EN(PHI2), .D(not_15_out), .Q(sbadd_latch_q));  // open: NOT_Q
  D_Latch adladd_latch (.EN(PHI2), .D(nor_3_out), .Q(adladd_latch_q));  // open: NOT_Q
  D_Latch ands_latch1 (.EN(PHI2), .D(AND), .NOT_Q(ands_latch1_not_q));  // open: Q
  D_Latch eors_latch1 (.EN(PHI2), .D(D29), .NOT_Q(eors_latch1_not_q));  // open: Q
  D_Latch ors_latch1 (.EN(PHI2), .D(not_5_out), .NOT_Q(ors_latch1_not_q));  // open: Q
  D_Latch srs_latch1 (.EN(PHI2), .D(SR), .NOT_Q(srs_latch1_not_q));  // open: Q
  D_Latch sums_latch1 (.EN(PHI2), .D(nor_17_out), .NOT_Q(sums_latch1_not_q));  // open: Q
  D_Latch daa_latch1 (.EN(PHI2), .D(not_13_out), .NOT_Q(daa_latch1_not_q));  // open: Q
  D_Latch addsb7_latch (.EN(PHI2), .D(nor_18_out), .Q(addsb7_latch_q));  // open: NOT_Q
  D_Latch addsb06_latch (.EN(PHI2), .D(nor_16_out), .NOT_Q(addsb06_latch_not_q));  // open: Q
  D_Latch addadl_latch (.EN(PHI2), .D(not_12_out), .NOT_Q(addadl_latch_not_q));  // open: Q
  D_Latch dsa_latch1 (.EN(PHI2), .D(nand_4_out), .NOT_Q(dsa_latch1_not_q));  // open: Q
  nor nor_19 (nor_19_out, ndbadd_latch_q, PHI2);
  nor nor_20 (nor_20_out, dbadd_latch_q, PHI2);
  nor nor_21 (nor_21_out, zadd_latch_q, PHI2);
  nor nor_22 (nor_22_out, sbadd_latch_q, PHI2);
  nor nor_23 (nor_23_out, adladd_latch_q, PHI2);
  D_Latch ands_latch2 (.EN(PHI1), .D(ands_latch1_not_q), .NOT_Q(ands_latch2_not_q));  // open: Q
  buf buffer_1 (ANDS, ands_latch2_not_q);
  D_Latch eors_latch2 (.EN(PHI1), .D(eors_latch1_not_q), .NOT_Q(eors_latch2_not_q));  // open: Q
  buf buffer_2 (EORS, eors_latch2_not_q);
  D_Latch ors_latch2 (.EN(PHI1), .D(ors_latch1_not_q), .NOT_Q(ors_latch2_not_q));  // open: Q
  buf buffer_3 (ORS, ors_latch2_not_q);
  D_Latch acin_latch5 (.EN(PHI1), .D(nor_15_out), .NOT_Q(acin_latch5_not_q));  // open: Q
  not not_16 (n_ACIN, acin_latch5_not_q);
  D_Latch srs_latch2 (.EN(PHI1), .D(srs_latch1_not_q), .NOT_Q(srs_latch2_not_q));  // open: Q
  buf buffer_4 (SRS, srs_latch2_not_q);
  D_Latch sums_latch2 (.EN(PHI1), .D(sums_latch1_not_q), .NOT_Q(sums_latch2_not_q));  // open: Q
  buf buffer_5 (SUMS, sums_latch2_not_q);
  D_Latch daa_latch2 (.EN(PHI1), .D(daa_latch1_not_q), .NOT_Q(daa_latch2_not_q));  // open: Q
  buf buffer_6 (n_DAA, daa_latch2_not_q);
  buf buffer_7 (ADD_SB7, addsb7_latch_q);
  buf buffer_8 (ADD_SB06, addsb06_latch_not_q);
  buf buffer_9 (ADD_ADL, addadl_latch_not_q);
  D_Latch dsa_latch2 (.EN(PHI1), .D(dsa_latch1_not_q), .NOT_Q(n_DSA));  // open: Q
  buf buffer_10 (NDB_ADD, nor_19_out);
  buf buffer_11 (DB_ADD, nor_20_out);
  buf buffer_12 (Z_ADD, nor_21_out);
  buf buffer_13 (SB_ADD, nor_22_out);
  buf buffer_14 (ADL_ADD, nor_23_out);

  // Other names for the same wires on the sheet: JSR_5 = D56; RTI_5 = D26; RTS_5 = D84; SBC0 = D51

  // Notes on the sheet:
  //   ROR
  //   EOR
  //   STK2
  //   RET
  //   JSR2
  //   D93
  //   OR
  //   NOADL
  //   D_OUT
  //   #ADL/ADD
  //   BRX
  //   SB/ADD
  //   CSET
  //   PGX
  //   /ACIN
  //   #NDB/ADD
  //   #ADD/SB7
  //   #ADD/SB06
  //   #ADL/ADD
  //   care!
endmodule

module BRANCH_LOGIC (
  input  n_IR5,
  input  D121,
  input  D126,
  input  n_C_OUT,
  input  n_V_OUT,
  input  n_N_OUT,
  input  n_Z_OUT,
  input  PHI1,
  input  PHI2,
  input  DB7_in,
  input  BR2,
  output n_BRTAKEN,
  output BRFW
);

  wire br2_latch_q, brfw_latch1_not_q, brfw_latch2_q, multiplexer_1_out, nor_1_out, nor_2_out, nor_3_out,
       nor_4_out, nor_5_out, not_1_out, not_2_out, not_3_out, not_4_out, not_5_out, not_6_out;

  not not_1 (not_1_out, D121);
  not not_2 (not_2_out, D126);
  not not_3 (not_3_out, D126);
  not not_4 (not_4_out, D121);
  nor nor_1 (nor_1_out, n_C_OUT, D126, not_1_out);
  nor nor_2 (nor_2_out, n_V_OUT, D121, not_2_out);
  nor nor_3 (nor_3_out, n_N_OUT, not_3_out, not_4_out);
  nor nor_4 (nor_4_out, D126, D121, n_Z_OUT);
  not not_5 (not_5_out, DB7_in);
  D_Latch br2_latch (.EN(PHI2), .D(BR2), .Q(br2_latch_q));  // open: NOT_Q
  D_Latch brfw_latch2 (.EN(PHI2), .D(brfw_latch1_not_q), .Q(brfw_latch2_q));  // open: NOT_Q
  nor nor_5 (nor_5_out, nor_1_out, nor_2_out, nor_3_out, nor_4_out);
  not not_6 (not_6_out, multiplexer_1_out);
  Multiplexer multiplexer_1 (.in0(brfw_latch2_q), .in1(not_5_out), .out(multiplexer_1_out), .sel(br2_latch_q));
  xor xor_1 (n_BRTAKEN, n_IR5, nor_5_out);
  D_Latch brfw_latch1 (.EN(PHI1), .D(not_6_out), .NOT_Q(brfw_latch1_not_q));  // open: Q
  not not_7 (BRFW, brfw_latch1_not_q);

  // Notes on the sheet:
  //   /IR6
  //   /IR7
  //   2-MUX
  //   BRFW_FF
endmodule

// PROGRAM COUNTER SETUP
module PC_SETUP (
  input  PHI1,
  input  PHI2,
  input  D56,
  input  D77,
  input  D78,
  input  D83,
  input  D84,
  input  D94,
  input  D95,
  input  D96,
  input  D129,
  input  n_ready,
  input  BR3,
  input  BR2,
  input  T0,
  input  T1,
  input  BR0,
  output PCL_DB,
  output PCH_DB,
  output PC_DB,
  output PCL_ADL,
  output PCH_ADH,
  output PCL_PCL,
  output ADL_PCL,
  output n_ADL_PCL,
  output DL_PCH,
  output ADH_PCH,
  output PCH_PCH,
  output n_PCH_PCH
);

  wire adh_pch_latch_q, adl_pcl_latch_q, and_1_out, and_2_out, nor_1_out, nor_2_out, nor_3_out, nor_4_out,
       nor_5_out, nor_8_out, nor_9_out, nor_10_out, nor_11_out, nor_12_out, nor_13_out, nor_14_out,
       nor_15_out, not_1_out, not_2_out, not_3_out, not_5_out, nready_latch_q, pch_adh_latch_not_q,
       pch_db_latch1_q, pch_db_latch2_not_q, pch_pch_latch_q, pcl_adl_latch_not_q, pcl_db_latch1_not_q,
       pcl_db_latch2_not_q, pcl_pcl_latch_q;

  nor nor_1 (nor_1_out, D77, D78);
  and and_1 (and_1_out, D83, ~D129);  // AND_Gate
  nor nor_2 (nor_2_out, D94, D95, D96);
  D_Latch pch_db_latch1 (.EN(PHI2), .D(nor_1_out), .Q(pch_db_latch1_q));  // open: NOT_Q
  D_Latch nready_latch (.EN(PHI1), .D(n_ready), .Q(nready_latch_q));  // open: NOT_Q
  nor nor_3 (nor_3_out, pch_db_latch1_q, n_ready);
  nor nor_4 (nor_4_out, nor_2_out, nready_latch_q);
  not not_1 (not_1_out, nready_latch_q);
  not not_2 (not_2_out, T0);
  nor nor_5 (nor_5_out, nor_4_out, not_2_out);
  and and_2 (and_2_out, not_1_out, BR3);
  nor nor_6 (DL_PCH, not_2_out, nor_2_out);
  D_Latch pcl_db_latch1 (.EN(PHI1), .D(nor_3_out), .NOT_Q(pcl_db_latch1_not_q));  // open: Q
  not not_3 (not_3_out, nor_8_out);
  nor nor_7 (n_ADL_PCL, not_3_out, D84, T0, and_2_out);
  nand nand_1 (PC_DB, pcl_db_latch1_not_q, nor_1_out);
  nor nor_8 (nor_8_out, T1, D56, and_1_out, nor_5_out, BR2);
  nor nor_9 (nor_9_out, D84, and_1_out, T0, T1, BR2, BR3);
  nor nor_10 (nor_10_out, nor_8_out, DL_PCH, BR0);
  not not_4 (n_PCH_PCH, nor_9_out);
  nor nor_11 (nor_11_out, nor_10_out, BR3);
  not not_5 (not_5_out, n_ADL_PCL);
  D_Latch pcl_db_latch2 (.EN(PHI2), .D(pcl_db_latch1_not_q), .NOT_Q(pcl_db_latch2_not_q));  // open: Q
  D_Latch pch_db_latch2 (.EN(PHI2), .D(nor_1_out), .NOT_Q(pch_db_latch2_not_q));  // open: Q
  D_Latch pcl_adl_latch (.EN(PHI2), .D(nor_8_out), .NOT_Q(pcl_adl_latch_not_q));  // open: Q
  D_Latch pch_adh_latch (.EN(PHI2), .D(nor_11_out), .NOT_Q(pch_adh_latch_not_q));  // open: Q
  D_Latch pcl_pcl_latch (.EN(PHI2), .D(not_5_out), .Q(pcl_pcl_latch_q));  // open: NOT_Q
  D_Latch adl_pcl_latch (.EN(PHI2), .D(n_ADL_PCL), .Q(adl_pcl_latch_q));  // open: NOT_Q
  D_Latch adh_pch_latch (.EN(PHI2), .D(nor_9_out), .Q(adh_pch_latch_q));  // open: NOT_Q
  D_Latch pch_pch_latch (.EN(PHI2), .D(n_PCH_PCH), .Q(pch_pch_latch_q));  // open: NOT_Q
  nor nor_12 (nor_12_out, pcl_pcl_latch_q, PHI2);
  nor nor_13 (nor_13_out, adl_pcl_latch_q, PHI2);
  nor nor_14 (nor_14_out, adh_pch_latch_q, PHI2);
  nor nor_15 (nor_15_out, pch_pch_latch_q, PHI2);
  buf buffer_1 (PCL_DB, pcl_db_latch2_not_q);
  buf buffer_2 (PCH_DB, pch_db_latch2_not_q);
  buf buffer_3 (PCL_ADL, pcl_adl_latch_not_q);
  buf buffer_4 (PCH_ADH, pch_adh_latch_not_q);
  buf buffer_5 (PCL_PCL, nor_12_out);
  buf buffer_6 (ADL_PCL, nor_13_out);
  buf buffer_7 (ADH_PCH, nor_14_out);
  buf buffer_8 (PCH_PCH, nor_15_out);

  // Other names for the same wires on the sheet: RTS_5 = D84

  // Notes on the sheet:
  //   JSR/5
  //   Push/pull
  //   JB
  //   #PCH/DB
  //   ABS/2
  //   DL/PCH
  //   #PCL/DB
  //   PC/DB
  //   DL/PCH
  //   #PCL/ADL
  //   #ADL/PCL
  //   #ADH/PCH
endmodule

module DISPATCH (
  input  PHI1,
  input  PHI2,
  input  BRK6E,
  input  BR2,
  input  RESP,
  input  ACR,
  input  DORES,
  input  PC_DB,
  input  D91,
  input  D92,
  input  BR3,
  input  D96,
  input  D97,
  input  D98,
  input  D100,
  input  D101,
  input  D102,
  input  D103,
  input  D104,
  input  D105,
  input  D106,
  input  D107,
  input  D111,
  input  D122,
  input  D123,
  input  D124,
  input  D125,
  input  RDY,
  input  B_OUT,
  input  BRFW,
  input  n_BRTAKEN,
  input  n_TWOCYCLE,
  input  n_ADL_PCL,
  input  n_IMPLIED,
  output ACRL2,
  output T6,
  output T7,
  output TRES2,
  output STOR,
  output Z_IR,
  output FETCH,
  output n_ready,
  output WR,
  output T1,
  output n_T0,
  output T0,
  output n_T1X,
  output n_IPC
);

  wire acr_latch1_not_q, and_1_out, and_2_out, and_3_out, and_4_out, and_5_out, and_6_out, br_latch1_q,
       br_latch2_not_q, comp_latch1_q, comp_latch2_q, comp_latch3_q, ends_latch1_q, ends_latch2_q,
       fetch_latch_not_q, ipc_latch1_q, ipc_latch2_q, ipc_latch3_q, multiplexer_1_out, n_MemOP, n_SHIFT,
       n_TRESX, nand_1_out, nand_2_out, nor_1_out, nor_2_out, nor_5_out, nor_6_out, nor_7_out, nor_8_out,
       nor_9_out, nor_10_out, nor_11_out, nor_12_out, nor_13_out, nor_14_out, nor_15_out, nor_16_out,
       nor_17_out, nor_18_out, nor_20_out, nor_21_out, nor_22_out, nor_23_out, nor_24_out, nor_26_out,
       nor_27_out, nor_28_out, nor_29_out, nor_30_out, nor_31_out, not_1_out, not_2_out, not_3_out,
       not_4_out, not_5_out, not_6_out, not_7_out, not_8_out, not_9_out, not_10_out, not_11_out, not_12_out,
       not_14_out, NotReadyPhi1, nready_latch_q, or_1_out, rdydelay_latch1_not_q, ready_latch1_not_q,
       ready_latch2_q, step_latch1_q, step_latch2_q, t0_latch_q, t1x_latch_q, t6_latch2_q, t7_latch1_not_q,
       t7_latch2_not_q, t67_latch_q, tresx_latch1_q, tresx_latch2_not_q, wr_latch_q, xor_1_out;

  not not_1 (not_1_out, D97);
  nor nor_1 (nor_1_out, D91, D92);
  nor nor_2 (nor_2_out, D100, D101, D102, D103, D104, D105);
  nor nor_3 (n_SHIFT, D106, D107);
  nor nor_4 (n_MemOP, D111, D122, D123, D124, D125);
  nor nor_5 (nor_5_out, BR2, BR3);
  not not_2 (not_2_out, nor_5_out);
  not not_3 (not_3_out, n_IMPLIED);
  not not_4 (not_4_out, ACR);
  not not_5 (not_5_out, NotReadyPhi1);
  not not_6 (not_6_out, nor_2_out);
  and and_1 (and_1_out, n_BRTAKEN, BR2);
  and and_2 (and_2_out, n_BRTAKEN, BR2);
  nor nor_6 (nor_6_out, n_ADL_PCL, not_2_out);
  and and_3 (and_3_out, not_4_out, not_5_out);
  nor nor_7 (nor_7_out, not_5_out, ACRL2);
  nor nor_8 (nor_8_out, STOR, PC_DB, D98, D100, T7, T6);
  nor nor_9 (nor_9_out, T0, and_1_out);
  not not_7 (not_7_out, T1);
  not not_8 (not_8_out, BR3);
  D_Latch rdydelay_latch1 (.EN(PHI1), .D(n_ready), .NOT_Q(rdydelay_latch1_not_q));  // open: Q
  nor nor_10 (nor_10_out, and_2_out, nor_6_out);
  nor nor_11 (nor_11_out, and_3_out, nor_7_out);
  Multiplexer multiplexer_1 (.in0(nor_9_out), .in1(not_7_out), .out(multiplexer_1_out), .sel(n_ready));
  not not_9 (not_9_out, n_ready);
  nor nor_12 (nor_12_out, not_8_out, NotReadyPhi1);
  not not_10 (not_10_out, ACR);
  D_Latch acr_latch1 (.EN(PHI1), .D(nor_11_out), .NOT_Q(acr_latch1_not_q));  // open: Q
  D_Latch acr_latch2 (.EN(PHI2), .D(acr_latch1_not_q), .NOT_Q(ACRL2));  // open: Q
  D_Latch tresx_latch1 (.EN(PHI2), .D(nor_1_out), .Q(tresx_latch1_q));  // open: NOT_Q
  not not_11 (not_11_out, n_SHIFT);
  nor nor_13 (nor_13_out, D96, not_11_out, n_MemOP);
  D_Latch wr_latch (.EN(PHI2), .D(nor_8_out), .Q(wr_latch_q));  // open: NOT_Q
  D_Latch ends_latch1 (.EN(PHI2), .D(multiplexer_1_out), .Q(ends_latch1_q));  // open: NOT_Q
  D_Latch ends_latch2 (.EN(PHI2), .D(RESP), .Q(ends_latch2_q));  // open: NOT_Q
  D_Latch nready_latch (.EN(PHI1), .D(not_9_out), .Q(nready_latch_q));  // open: NOT_Q
  D_Latch br_latch2 (.EN(PHI2), .D(nor_12_out), .NOT_Q(br_latch2_not_q));  // open: Q
  xor xor_1 (xor_1_out, BRFW, not_10_out);
  D_Latch rdydelay_latch2 (.EN(PHI2), .D(rdydelay_latch1_not_q), .NOT_Q(NotReadyPhi1));  // open: Q
  D_Latch comp_latch1 (.EN(PHI1), .D(not_14_out), .Q(comp_latch1_q));  // open: NOT_Q
  D_Latch comp_latch2 (.EN(PHI1), .D(n_TWOCYCLE), .Q(comp_latch2_q));  // open: NOT_Q
  D_Latch comp_latch3 (.EN(PHI1), .D(n_TRESX), .Q(comp_latch3_q));  // open: NOT_Q
  D_Latch br_latch1 (.EN(PHI2), .D(nor_10_out), .Q(br_latch1_q));  // open: NOT_Q
  nand nand_1 (nand_1_out, n_SHIFT, not_1_out);
  nor nor_14 (nor_14_out, ends_latch1_q, ends_latch2_q);
  and and_4 (and_4_out, ~br_latch2_not_q, xor_1_out);  // AND_Gate
  and and_5 (and_5_out, comp_latch2_q, comp_latch3_q);
  nor nor_15 (nor_15_out, nor_13_out, T7, not_6_out, BR3);
  nor nor_16 (nor_16_out, n_SHIFT, n_MemOP, n_ready);
  not not_12 (not_12_out, n_ready);
  nor nor_17 (nor_17_out, nor_11_out, tresx_latch1_q, n_ready, nand_1_out);
  nor nor_18 (nor_18_out, RDY, ready_latch2_q);
  nor nor_19 (WR, n_ready, wr_latch_q, DORES);
  nor nor_20 (nor_20_out, nready_latch_q, RESP, step_latch2_q);
  nor nor_21 (nor_21_out, step_latch1_q, and_4_out);
  nor nor_22 (nor_22_out, nor_21_out, n_ready);
  nor nor_23 (nor_23_out, nor_22_out, nor_14_out);
  nor nor_24 (nor_24_out, comp_latch1_q, and_5_out);
  nor nor_25 (n_T0, nor_24_out, nor_26_out);
  nor nor_26 (nor_26_out, t0_latch_q, t1x_latch_q);
  nor nor_27 (nor_27_out, t0_latch_q, n_ready);
  nor nor_28 (nor_28_out, n_ready, br_latch1_q, not_3_out);
  and and_6 (and_6_out, t6_latch2_q, n_ready);
  D_Latch t67_latch (.EN(PHI2), .D(nor_16_out), .Q(t67_latch_q));  // open: NOT_Q
  nand nand_2 (nand_2_out, T6, not_12_out);
  nor nor_29 (nor_29_out, RESP, nor_14_out, nor_30_out);
  nor nor_30 (nor_30_out, n_ready, nor_15_out);
  nor nor_31 (nor_31_out, and_6_out, t67_latch_q);
  D_Latch t7_latch1 (.EN(PHI2), .D(nand_2_out), .NOT_Q(t7_latch1_not_q));  // open: Q
  nor nor_32 (n_TRESX, nor_17_out, BRK6E, tresx_latch2_not_q);
  D_Latch tresx_latch2 (.EN(PHI2), .D(nor_29_out), .NOT_Q(tresx_latch2_not_q));  // open: Q
  D_Latch fetch_latch (.EN(PHI2), .D(T1), .NOT_Q(fetch_latch_not_q));  // open: Q
  D_Latch ready_latch1 (.EN(PHI2), .D(nor_18_out), .NOT_Q(ready_latch1_not_q));  // open: Q
  not not_13 (n_ready, ready_latch1_not_q);
  D_Latch ready_latch2 (.EN(PHI1), .D(WR), .Q(ready_latch2_q));  // open: NOT_Q
  D_Latch step_latch1 (.EN(PHI2), .D(nor_20_out), .Q(step_latch1_q));  // open: NOT_Q
  D_Latch step_latch2 (.EN(PHI1), .D(nor_21_out), .Q(step_latch2_q));  // open: NOT_Q
  D_Latch t1_latch (.EN(PHI1), .D(nor_23_out), .NOT_Q(T1));  // open: Q
  not not_14 (not_14_out, nor_23_out);
  D_Latch t0_latch (.EN(PHI2), .D(n_T0), .Q(t0_latch_q));  // open: NOT_Q
  D_Latch t1x_latch (.EN(PHI1), .D(nor_27_out), .Q(t1x_latch_q), .NOT_Q(n_T1X));
  D_Latch ipc_latch1 (.EN(PHI1), .D(B_OUT), .Q(ipc_latch1_q));  // open: NOT_Q
  D_Latch ipc_latch2 (.EN(PHI1), .D(and_4_out), .Q(ipc_latch2_q));  // open: NOT_Q
  D_Latch ipc_latch3 (.EN(PHI1), .D(nor_28_out), .Q(ipc_latch3_q));  // open: NOT_Q
  D_Latch t6_latch2 (.EN(PHI2), .D(T6), .Q(t6_latch2_q));  // open: NOT_Q
  D_Latch t6_latch1 (.EN(PHI1), .D(nor_31_out), .NOT_Q(T6));  // open: Q
  D_Latch t7_latch2 (.EN(PHI1), .D(t7_latch1_not_q), .NOT_Q(t7_latch2_not_q));  // open: Q
  D_Latch tres2_latch (.EN(PHI1), .D(n_TRESX), .NOT_Q(TRES2));  // open: Q
  nor nor_33 (STOR, n_MemOP, not_1_out);
  nor nor_34 (FETCH, fetch_latch_not_q, n_ready);
  not not_15 (T0, n_T0);
  or or_1 (or_1_out, ipc_latch2_q, ipc_latch3_q);
  not not_16 (T7, t7_latch2_not_q);
  nand nand_3 (Z_IR, B_OUT, FETCH);
  nand nand_4 (n_IPC, ipc_latch1_q, or_1_out);

  // Notes on the sheet:
  //   /STORE
  //   ACRL_FF
  //   STOR
  //   ReadyDelay
  //   ACRL1
  //   REST
  //   ENDS
  //   ENDS
  //   ENDS
  //   ENDX
  //   RDY
  //   STEP_FF
  //   T6_FF
  //   RDY_FF
  //   WR
  //   T0_FF
  //   TRES1
endmodule

// BUS CONTROL
module BUS_CONTROL (
  input  PHI1,
  input  PHI2,
  input  n_SBXY,
  input  D55,
  input  D57,
  input  D58,
  input  D59,
  input  D60,
  input  D61,
  input  D62,
  input  D63,
  input  D64,
  input  D65,
  input  D66,
  input  D67,
  input  D68,
  input  AND,
  input  D71,
  input  D72,
  input  D73,
  input  D74,
  input  D79,
  input  STOR,
  input  D81,
  input  D82,
  input  D84,
  input  D89,
  input  D90,
  input  D91,
  input  D83,
  input  D128,
  input  D129,
  input  Z_ADL0,
  input  BR2,
  input  ACRL2,
  input  DL_PCH,
  input  BR3,
  input  n_ready,
  input  T2,
  input  INC_SB,
  input  D45,
  input  BRK6E,
  input  D46,
  input  D47,
  input  D48,
  input  STXY,
  input  D101,
  input  n_PCH_PCH,
  input  T0,
  input  T1,
  input  T6,
  input  T7,
  input  D56,
  output Z_ADH0,
  output Z_ADH17,
  output SB_AC,
  output ZTST,
  output ADL_ABL,
  output AC_SB,
  output SB_DB,
  output AC_DB,
  output PGX,
  output SB_ADH,
  output DL_ADH,
  output DL_ADL,
  output ADH_ABH,
  output DL_DB
);

  wire ac_db_latch_q, ac_sb_latch_q, adh_abh_latch_not_q, adl_abl_latch_not_q, and_1_out, and_2_out,
       and_3_out, and_4_out, and_5_out, and_6_out, dl_adh_latch_not_q, dl_adl_latch_not_q, dl_db_latch_not_q,
       nand_2_out, nand_3_out, nand_4_out, nand_5_out, nor_1_out, nor_2_out, nor_3_out, nor_4_out, nor_5_out,
       nor_6_out, nor_7_out, nor_8_out, nor_9_out, nor_10_out, nor_11_out, nor_12_out, nor_13_out,
       nor_14_out, nor_15_out, nor_16_out, nor_17_out, nor_18_out, nor_19_out, nor_20_out, nor_21_out,
       nor_22_out, nor_23_out, nor_24_out, nor_25_out, not_1_out, not_2_out, not_3_out, not_4_out, not_5_out,
       not_6_out, not_7_out, not_8_out, not_9_out, nready_latch_not_q, or_1_out, sb_ac_latch_q,
       sb_adh_latch_not_q, sb_db_latch_not_q, z_adh17_latch_not_q;

  not not_1 (not_1_out, D64);
  nor nor_1 (nor_1_out, D71, D72);
  not not_2 (not_2_out, D73);
  and and_1 (and_1_out, D79, STOR);
  nor nor_2 (nor_2_out, D81, D82);
  and and_2 (and_2_out, D90, ~D129);  // AND_Gate
  and and_3 (and_3_out, D83, ~D129);  // AND_Gate
  and and_4 (and_4_out, D128, ~D129);  // AND_Gate
  not not_3 (not_3_out, D48);
  nor nor_3 (nor_3_out, D58, D59, D60, D61, D62, D63, D64);
  and and_5 (and_5_out, not_1_out, D65);
  not not_4 (not_4_out, nor_1_out);
  nand nand_1 (PGX, nor_1_out, not_2_out);
  nor nor_4 (nor_4_out, D74, and_1_out);
  nor nor_5 (nor_5_out, D89, and_2_out, D91, D84);
  nor nor_6 (nor_6_out, and_3_out, T0);
  D_Latch nready_latch (.EN(PHI1), .D(n_ready), .NOT_Q(nready_latch_not_q));  // open: Q
  nor nor_7 (nor_7_out, INC_SB, D45, BRK6E, D46, D47, D48);
  not not_5 (not_5_out, nor_3_out);
  nor nor_8 (nor_8_out, and_5_out, D66, D67, D68, AND);
  not not_6 (not_6_out, nor_5_out);
  nor nor_9 (nor_9_out, nor_6_out, and_4_out);
  nand nand_2 (nand_2_out, ACRL2, nready_latch_not_q);
  not not_7 (not_7_out, nor_7_out);
  nand nand_3 (nand_3_out, not_3_out, STXY);
  nor nor_10 (nor_10_out, n_SBXY, not_5_out, T7, AND);
  nor nor_11 (nor_11_out, not_4_out, n_ready);
  nor nor_12 (nor_12_out, PGX, BR3);
  nor nor_13 (nor_13_out, not_6_out, T2, n_PCH_PCH, D56);
  nand nand_4 (nand_4_out, T6, D55);
  not not_8 (not_8_out, nand_4_out);
  not not_9 (not_9_out, nor_2_out);
  nor nor_14 (nor_14_out, nor_12_out, nand_2_out);
  nor nor_15 (nor_15_out, n_ready, nor_13_out);
  nor nor_16 (nor_16_out, D57, not_9_out);
  nor nor_17 (nor_17_out, nor_10_out, AND);
  or or_1 (or_1_out, nor_14_out, nor_15_out);
  nor nor_18 (nor_18_out, T7, T6);
  nand nand_5 (nand_5_out, nor_18_out, nor_11_out);
  nor nor_19 (nor_19_out, not_8_out, nor_17_out, D67, T1, BR2, nand_3_out);
  nor nor_20 (nor_20_out, DL_PCH, not_6_out);
  nor nor_21 (nor_21_out, Z_ADL0, and_6_out);
  and and_6 (and_6_out, or_1_out, ~BR3);  // AND_Gate
  nor nor_22 (nor_22_out, BR2, nor_9_out, not_7_out, D101, T6);
  D_Latch z_adh0_latch (.EN(PHI2), .D(nor_2_out), .NOT_Q(Z_ADH0));  // open: Q
  D_Latch z_adh17_latch (.EN(PHI2), .D(nor_16_out), .NOT_Q(z_adh17_latch_not_q));  // open: Q
  D_Latch sb_ac_latch (.EN(PHI2), .D(nor_3_out), .Q(sb_ac_latch_q));  // open: NOT_Q
  D_Latch adl_abl_latch (.EN(PHI2), .D(nand_5_out), .NOT_Q(adl_abl_latch_not_q));  // open: Q
  D_Latch ac_sb_latch (.EN(PHI2), .D(nor_8_out), .Q(ac_sb_latch_q));  // open: NOT_Q
  D_Latch sb_db_latch (.EN(PHI2), .D(nor_19_out), .NOT_Q(sb_db_latch_not_q));  // open: Q
  D_Latch ac_db_latch (.EN(PHI2), .D(nor_4_out), .Q(ac_db_latch_q));  // open: NOT_Q
  D_Latch sb_adh_latch (.EN(PHI2), .D(nor_12_out), .NOT_Q(sb_adh_latch_not_q));  // open: Q
  D_Latch dl_adh_latch (.EN(PHI2), .D(nor_20_out), .NOT_Q(dl_adh_latch_not_q));  // open: Q
  D_Latch dl_adl_latch (.EN(PHI2), .D(nor_2_out), .NOT_Q(dl_adl_latch_not_q));  // open: Q
  D_Latch adh_abh_latch (.EN(PHI2), .D(nor_21_out), .NOT_Q(adh_abh_latch_not_q));  // open: Q
  D_Latch dl_db_latch (.EN(PHI2), .D(nor_22_out), .NOT_Q(dl_db_latch_not_q));  // open: Q
  buf buffer_1 (Z_ADH17, z_adh17_latch_not_q);
  buf buffer_2 (SB_AC, nor_23_out);
  nor nor_23 (nor_23_out, sb_ac_latch_q, PHI2);
  not not_10 (ZTST, nor_10_out);
  buf buffer_3 (ADL_ABL, adl_abl_latch_not_q);
  buf buffer_4 (AC_SB, nor_24_out);
  nor nor_24 (nor_24_out, ac_sb_latch_q, PHI2);
  buf buffer_5 (SB_DB, sb_db_latch_not_q);
  buf buffer_6 (AC_DB, nor_25_out);
  nor nor_25 (nor_25_out, ac_db_latch_q, PHI2);
  buf buffer_7 (SB_ADH, sb_adh_latch_not_q);
  buf buffer_8 (DL_ADH, dl_adh_latch_not_q);
  buf buffer_9 (DL_ADL, dl_adl_latch_not_q);
  buf buffer_10 (ADH_ABH, adh_abh_latch_not_q);
  buf buffer_11 (DL_DB, dl_db_latch_not_q);

  // Other names for the same wires on the sheet: RTS_5 = D84

  // Notes on the sheet:
  //   BR0
  //   STA
  //   push/pull
  //   JSR2
  //   ABS/2
  //   #DL/ADL
  //   IMPLIED
  //   #SBXY
  //   #SB/AC
  //   PGX
  //   IND
  //   JSR/5
  //   #DL/ADL
  //   AND
  //   #ZTST
  //   SBA
  //   JSXY
  //   JMP/4
  //   JSXY
  //   #DL/ADL
  //   #SB/AC
  //   #ADL/ABL
  //   #AC/SB
  //   #SB/DB
  //   #DL/ADL
  //   #DL/DB
endmodule

// FLAGS CONTROL
module FLAGS_CONTROL (
  input  PHI2,
  input  D98,
  input  D99,
  input  D108,
  input  D110,
  input  D120,
  input  D127,
  input  D107,
  input  T7,
  input  D112,
  input  D116,
  input  D117,
  input  D118,
  input  D119,
  input  ZTST,
  input  D109,
  input  n_ready,
  input  SR,
  input  D114,
  input  D115,
  input  D113,
  output P_DB,
  output IR5_I,
  output IR5_C,
  output IR5_D,
  output Z_V,
  output ACR_C,
  output DBZ_Z,
  output DB_N,
  output DB_P,
  output DB_C,
  output DB_V
);

  wire and_1_out, and_2_out, bit_latch_q, dbn_latch_q, dbz_latch_q, nor_1_out, nor_2_out, nor_3_out,
       nor_4_out, nor_5_out, not_1_out, not_2_out, not_3_out, not_4_out, not_5_out, pin_latch_q;

  nor nor_1 (nor_1_out, D98, D99);
  not not_1 (not_1_out, D108);
  not not_2 (not_2_out, D110);
  not not_3 (not_3_out, D120);
  not not_4 (not_4_out, D127);
  and and_1 (and_1_out, D107, T7);
  nor nor_2 (nor_2_out, D114, D115);
  not not_5 (not_5_out, D113);
  nor nor_3 (nor_3_out, and_1_out, D112, D116, D117, D118, D119);
  nor nor_4 (nor_4_out, ACR_C, ZTST, D109);
  nor nor_5 (nor_5_out, SR, DB_P);
  D_Latch pdb_latch (.EN(PHI2), .D(nor_1_out), .NOT_Q(P_DB));  // open: Q
  D_Latch iri_latch (.EN(PHI2), .D(not_1_out), .NOT_Q(IR5_I));  // open: Q
  D_Latch irc_latch (.EN(PHI2), .D(not_2_out), .NOT_Q(IR5_C));  // open: Q
  D_Latch ird_latch (.EN(PHI2), .D(not_3_out), .NOT_Q(IR5_D));  // open: Q
  D_Latch zv_latch (.EN(PHI2), .D(not_4_out), .NOT_Q(Z_V));  // open: Q
  D_Latch acrc_latch (.EN(PHI2), .D(nor_3_out), .NOT_Q(ACR_C));  // open: Q
  D_Latch dbz_latch (.EN(PHI2), .D(nor_4_out), .Q(dbz_latch_q), .NOT_Q(DBZ_Z));
  D_Latch dbn_latch (.EN(PHI2), .D(D109), .Q(dbn_latch_q));  // open: NOT_Q
  D_Latch dbc_latch (.EN(PHI2), .D(nor_5_out), .NOT_Q(DB_C));  // open: Q
  D_Latch pin_latch (.EN(PHI2), .D(nor_2_out), .Q(pin_latch_q));  // open: NOT_Q
  D_Latch bit_latch (.EN(PHI2), .D(not_5_out), .Q(bit_latch_q));  // open: NOT_Q
  and and_2 (and_2_out, dbz_latch_q, pin_latch_q);
  nor nor_6 (DB_P, pin_latch_q, n_ready);
  nand nand_1 (DB_V, pin_latch_q, bit_latch_q);
  nor nor_7 (DB_N, and_2_out, dbn_latch_q);

  // Notes on the sheet:
  //   AVR/V
  //   BIT1
  //   BIT0
  //   /POUT
  //   /CSI
  //   /PIN
  //   /ARIT
  //   ZTST
  //   BIT1
endmodule

module FLAGS (
  input  P_DB,
  input  B_OUT,
  input  DB0,
  input  DB1,
  input  DB2,
  input  DB3,
  input  DB4,
  input  DB5,
  input  DB6,
  input  DB7,
  input  DB_P,
  input  DBZ_Z,
  input  DB_N,
  input  IR5_C,
  input  ACR,
  input  DB_C,
  input  ACR_C,
  input  IR5_D,
  input  PHI1,
  input  PHI2,
  input  n_IR5,
  input  IR5_I,
  input  BRK6E,
  input  AVR,
  input  DB_V,
  input  D112,
  input  Z_V,
  input  SO,
  output DB_out0,
  output DB_out1,
  output DB_out2,
  output DB_out3,
  output DB_out4,
  output DB_out5,
  output DB_out6,
  output DB_out7,
  output n_Z_OUT,
  output n_N_OUT,
  output n_C_OUT,
  output n_D_OUT,
  output n_I_OUT,
  output n_V_OUT
);

  wire and_1_out, and_2_out, and_3_out, and_4_out, and_5_out, and_6_out, and_7_out, and_8_out, and_9_out,
       and_10_out, and_11_out, and_12_out, and_13_out, and_14_out, and_15_out, and_16_out, and_17_out,
       and_18_out, avr_latch_q, c_latch2_q, d_latch2_q, i_latch1_not_q, i_latch2_q, n_latch2_q, nor_1_out,
       nor_2_out, nor_3_out, nor_4_out, nor_5_out, nor_6_out, nor_7_out, nor_8_out, nor_9_out, nor_10_out,
       nor_11_out, nor_12_out, nor_13_out, not_1_out, not_2_out, not_3_out, not_4_out, not_5_out, not_6_out,
       not_7_out, not_8_out, not_9_out, not_10_out, not_11_out, not_12_out, not_13_out, not_14_out,
       not_15_out, not_16_out, not_17_out, so_latch1_not_q, so_latch2_not_q, so_latch3_q, v_latch2_q,
       vset_latch_q, z_latch2_q;

  D_Latch avr_latch (.EN(PHI2), .D(D112), .Q(avr_latch_q));  // open: NOT_Q
  not not_1 (not_1_out, SO);
  nor nor_1 (nor_1_out, DB0, DB1, DB2, DB3, DB4, DB5, DB6, DB7);
  not not_2 (not_2_out, DB1);
  not not_3 (not_3_out, nor_1_out);
  not not_4 (not_4_out, DB7);
  nor nor_2 (nor_2_out, DB_P, DBZ_Z);
  not not_5 (not_5_out, DB_N);
  not not_6 (not_6_out, ACR);
  not not_7 (not_7_out, DB0);
  nor nor_3 (nor_3_out, DB_C, IR5_C, ACR_C);
  not not_8 (not_8_out, DB3);
  nor nor_4 (nor_4_out, IR5_D, DB_P);
  not not_9 (not_9_out, DB2);
  nor nor_5 (nor_5_out, DB_P, IR5_I);
  not not_10 (not_10_out, AVR);
  not not_11 (not_11_out, DB6);
  nor nor_6 (nor_6_out, DB_V, avr_latch_q, vset_latch_q);
  D_Latch so_latch1 (.EN(PHI1), .D(not_1_out), .NOT_Q(so_latch1_not_q));  // open: Q
  and and_1 (and_1_out, not_2_out, DB_P);
  and and_2 (and_2_out, not_3_out, DBZ_Z);
  and and_3 (and_3_out, nor_2_out, z_latch2_q);
  and and_4 (and_4_out, not_4_out, DB_N);
  and and_5 (and_5_out, not_5_out, n_latch2_q);
  and and_6 (and_6_out, n_IR5, IR5_C);
  and and_7 (and_7_out, not_6_out, ACR_C);
  and and_8 (and_8_out, not_7_out, DB_C);
  and and_9 (and_9_out, nor_3_out, c_latch2_q);
  and and_10 (and_10_out, IR5_D, n_IR5);
  and and_11 (and_11_out, not_8_out, DB_P);
  and and_12 (and_12_out, nor_4_out, d_latch2_q);
  and and_13 (and_13_out, n_IR5, IR5_I);
  and and_14 (and_14_out, not_9_out, DB_P);
  and and_15 (and_15_out, nor_5_out, i_latch2_q);
  and and_16 (and_16_out, not_10_out, avr_latch_q);
  and and_17 (and_17_out, not_11_out, DB_V);
  and and_18 (and_18_out, nor_6_out, v_latch2_q);
  D_Latch so_latch2 (.EN(PHI2), .D(so_latch1_not_q), .NOT_Q(so_latch2_not_q));  // open: Q
  nor nor_7 (nor_7_out, and_1_out, and_2_out, and_3_out);
  nor nor_8 (nor_8_out, and_4_out, and_5_out);
  nor nor_9 (nor_9_out, and_6_out, and_7_out, and_8_out, and_9_out);
  nor nor_10 (nor_10_out, and_10_out, and_11_out, and_12_out);
  nor nor_11 (nor_11_out, and_13_out, and_14_out, and_15_out);
  nor nor_12 (nor_12_out, and_16_out, and_17_out, and_18_out, Z_V);
  D_Latch so_latch3 (.EN(PHI1), .D(so_latch2_not_q), .Q(so_latch3_q));  // open: NOT_Q
  nor nor_13 (nor_13_out, so_latch3_q, so_latch1_not_q);
  D_Latch z_latch1 (.EN(PHI1), .D(nor_7_out), .NOT_Q(n_Z_OUT));  // open: Q
  D_Latch z_latch2 (.EN(PHI2), .D(n_Z_OUT), .Q(z_latch2_q));  // open: NOT_Q
  D_Latch n_latch1 (.EN(PHI1), .D(nor_8_out), .NOT_Q(n_N_OUT));  // open: Q
  D_Latch n_latch2 (.EN(PHI2), .D(n_N_OUT), .Q(n_latch2_q));  // open: NOT_Q
  D_Latch c_latch1 (.EN(PHI1), .D(nor_9_out), .NOT_Q(n_C_OUT));  // open: Q
  D_Latch c_latch2 (.EN(PHI2), .D(n_C_OUT), .Q(c_latch2_q));  // open: NOT_Q
  D_Latch d_latch1 (.EN(PHI1), .D(nor_10_out), .NOT_Q(n_D_OUT));  // open: Q
  D_Latch d_latch2 (.EN(PHI2), .D(n_D_OUT), .Q(d_latch2_q));  // open: NOT_Q
  D_Latch i_latch1 (.EN(PHI1), .D(nor_11_out), .NOT_Q(i_latch1_not_q));  // open: Q
  D_Latch i_latch2 (.EN(PHI2), .D(n_I_OUT), .Q(i_latch2_q));  // open: NOT_Q
  D_Latch v_latch1 (.EN(PHI1), .D(nor_12_out), .NOT_Q(n_V_OUT));  // open: Q
  D_Latch v_latch2 (.EN(PHI2), .D(n_V_OUT), .Q(v_latch2_q));  // open: NOT_Q
  D_Latch vset_latch (.EN(PHI2), .D(nor_13_out), .Q(vset_latch_q));  // open: NOT_Q
  and and_19 (n_I_OUT, ~BRK6E, i_latch1_not_q);  // AND_Gate
  assign DB_out0 = P_DB ? not_12_out : 1'bz;  // Controlled_Buffer controlled_buffer_1
  not not_12 (not_12_out, n_C_OUT);
  assign DB_out1 = P_DB ? not_13_out : 1'bz;  // Controlled_Buffer controlled_buffer_2
  not not_13 (not_13_out, n_Z_OUT);
  assign DB_out2 = P_DB ? not_14_out : 1'bz;  // Controlled_Buffer controlled_buffer_3
  not not_14 (not_14_out, n_I_OUT);
  assign DB_out3 = P_DB ? not_15_out : 1'bz;  // Controlled_Buffer controlled_buffer_4
  not not_15 (not_15_out, n_D_OUT);
  assign DB_out4 = P_DB ? B_OUT : 1'bz;  // Controlled_Buffer controlled_buffer_5
  assign DB_out6 = P_DB ? not_16_out : 1'bz;  // Controlled_Buffer controlled_buffer_6
  not not_16 (not_16_out, n_V_OUT);
  assign DB_out7 = P_DB ? not_17_out : 1'bz;  // Controlled_Buffer controlled_buffer_7
  not not_17 (not_17_out, n_N_OUT);

  // Notes on the sheet:
  //   AVR/V
  //   ACR/C
  //   /DB1
  //   /DBZ
  //   /DB7
  //   DB/C
  //   IR5/D
  //   IR5/I
  //   DB/V
  //   1/V
  //   IR5/C
  //   /ACR
  //   ACR/C
  //   /DB0
  //   DB/C
  //   IR5/D
  //   /DB3
  //   IR5/I
  //   /DB2
  //   /AVR
  //   /DB6
  //   DB/V
  //   0/V
  //   SO_frompad
  //   Z FLAG
  //   /Z_OUT
  //   N FLAG
  //   /N_OUT
  //   C FLAG
  //   /C_OUT
  //   D FLAG
  //   /D_OUT
  //   I FLAG
  //   V FLAG
  //   /V_OUT
  //   /I_OUT
  //   N.C.
endmodule

module ABH (
  input  PHI1,
  input  PHI2,
  input  ADH_ABH,
  input  [7:0] ADH,
  output [7:0] A
);

  ABH_BIT _0 (.ADH_ABH(ADH_ABH), .ADHx(ADH[0]), .PHI1(PHI1), .PHI2(PHI2), .Ax(A[0]));
  ABH_BIT _1 (.ADH_ABH(ADH_ABH), .ADHx(ADH[1]), .PHI1(PHI1), .PHI2(PHI2), .Ax(A[1]));
  ABH_BIT _2 (.ADH_ABH(ADH_ABH), .ADHx(ADH[2]), .PHI1(PHI1), .PHI2(PHI2), .Ax(A[2]));
  ABH_BIT _3 (.ADH_ABH(ADH_ABH), .ADHx(ADH[3]), .PHI1(PHI1), .PHI2(PHI2), .Ax(A[3]));
  ABH_BIT _4 (.ADH_ABH(ADH_ABH), .ADHx(ADH[4]), .PHI1(PHI1), .PHI2(PHI2), .Ax(A[4]));
  ABH_BIT _5 (.ADH_ABH(ADH_ABH), .ADHx(ADH[5]), .PHI1(PHI1), .PHI2(PHI2), .Ax(A[5]));
  ABH_BIT _6 (.ADH_ABH(ADH_ABH), .ADHx(ADH[6]), .PHI1(PHI1), .PHI2(PHI2), .Ax(A[6]));
  ABH_BIT _7 (.ADH_ABH(ADH_ABH), .ADHx(ADH[7]), .PHI1(PHI1), .PHI2(PHI2), .Ax(A[7]));
endmodule

module ABL (
  input  PHI1,
  input  PHI2,
  input  ADL_ABL,
  input  [7:0] ADL,
  output [7:0] A
);

  ABL_BIT _0 (.ADL_ABL(ADL_ABL), .ADLx(ADL[0]), .PHI1(PHI1), .PHI2(PHI2), .Ax(A[0]));
  ABL_BIT _1 (.ADL_ABL(ADL_ABL), .ADLx(ADL[1]), .PHI1(PHI1), .PHI2(PHI2), .Ax(A[1]));
  ABL_BIT _2 (.ADL_ABL(ADL_ABL), .ADLx(ADL[2]), .PHI1(PHI1), .PHI2(PHI2), .Ax(A[2]));
  ABL_BIT _3 (.ADL_ABL(ADL_ABL), .ADLx(ADL[3]), .PHI1(PHI1), .PHI2(PHI2), .Ax(A[3]));
  ABL_BIT _4 (.ADL_ABL(ADL_ABL), .ADLx(ADL[4]), .PHI1(PHI1), .PHI2(PHI2), .Ax(A[4]));
  ABL_BIT _5 (.ADL_ABL(ADL_ABL), .ADLx(ADL[5]), .PHI1(PHI1), .PHI2(PHI2), .Ax(A[5]));
  ABL_BIT _6 (.ADL_ABL(ADL_ABL), .ADLx(ADL[6]), .PHI1(PHI1), .PHI2(PHI2), .Ax(A[6]));
  ABL_BIT _7 (.ADL_ABL(ADL_ABL), .ADLx(ADL[7]), .PHI1(PHI1), .PHI2(PHI2), .Ax(A[7]));
endmodule

module REGS_BIT (
  input  PHI2,
  input  Y_SB,
  input  SB_Y,
  input  X_SB,
  input  SB_X,
  input  S_ADL,
  input  S_S,
  input  SB_S,
  input  S_SB,
  input  SBx_in,
  output SBx_out,
  output ADLx,
  output Y_Debug,
  output X_Debug,
  output S_Debug
);

  wire and_1_out, and_2_out, multiplexer_1_out, not_1_out, not_2_out, not_3_out, S_in_not_q;

  not not_1 (not_1_out, PHI2);
  not not_2 (not_2_out, PHI2);
  not not_3 (not_3_out, PHI2);
  and and_1 (and_1_out, not_1_out, SB_Y);
  DFF_Level Y (.EN(and_1_out), .D(SBx_in), .Q(Y_Debug));  // open: NOT_Q
  and and_2 (and_2_out, not_2_out, SB_X);
  DFF_Level X (.EN(and_2_out), .D(SBx_in), .Q(X_Debug));  // open: NOT_Q
  Multiplexer multiplexer_1 (.in0(S_Debug), .in1(SBx_in), .out(multiplexer_1_out), .sel(SB_S));
  D_Latch S_in (.EN(not_3_out), .D(multiplexer_1_out), .NOT_Q(S_in_not_q));  // open: Q
  D_Latch S_out (.EN(PHI2), .D(S_in_not_q), .NOT_Q(S_Debug));  // open: Q
  assign SBx_out = Y_SB ? Y_Debug : 1'bz;  // Controlled_Buffer controlled_buffer_1
  assign SBx_out = X_SB ? X_Debug : 1'bz;  // Controlled_Buffer controlled_buffer_2
  assign SBx_out = S_SB ? S_Debug : 1'bz;  // Controlled_Buffer controlled_buffer_3
  assign ADLx = S_ADL ? S_Debug : 1'bz;  // Controlled_Buffer controlled_buffer_4

  // Notes on the sheet:
  //   unused
endmodule

module REGS (
  input  PHI2,
  input  Y_SB,
  input  SB_Y,
  input  X_SB,
  input  SB_X,
  input  S_ADL,
  input  S_S,
  input  SB_S,
  input  S_SB,
  input  [7:0] SB_in,
  output [7:0] SB_out,
  output [7:0] ADL_out,
  output [7:0] S_Debug,
  output [7:0] Y_Debug,
  output [7:0] X_Debug
);

  REGS_BIT r0 (
    .Y_SB(Y_SB), .SB_Y(SB_Y), .X_SB(X_SB), .SB_X(SB_X), .S_ADL(S_ADL), .S_S(S_S), .SB_S(SB_S), .S_SB(S_SB),
    .SBx_in(SB_in[0]), .PHI2(PHI2), .ADLx(ADL_out[0]), .Y_Debug(Y_Debug[0]), .X_Debug(X_Debug[0]),
    .S_Debug(S_Debug[0]), .SBx_out(SB_out[0]));
  REGS_BIT r4 (
    .Y_SB(Y_SB), .SB_Y(SB_Y), .X_SB(X_SB), .SB_X(SB_X), .S_ADL(S_ADL), .S_S(S_S), .SB_S(SB_S), .S_SB(S_SB),
    .SBx_in(SB_in[4]), .PHI2(PHI2), .ADLx(ADL_out[4]), .Y_Debug(Y_Debug[4]), .X_Debug(X_Debug[4]),
    .S_Debug(S_Debug[4]), .SBx_out(SB_out[4]));
  REGS_BIT r1 (
    .Y_SB(Y_SB), .SB_Y(SB_Y), .X_SB(X_SB), .SB_X(SB_X), .S_ADL(S_ADL), .S_S(S_S), .SB_S(SB_S), .S_SB(S_SB),
    .SBx_in(SB_in[1]), .PHI2(PHI2), .ADLx(ADL_out[1]), .Y_Debug(Y_Debug[1]), .X_Debug(X_Debug[1]),
    .S_Debug(S_Debug[1]), .SBx_out(SB_out[1]));
  REGS_BIT r5 (
    .Y_SB(Y_SB), .SB_Y(SB_Y), .X_SB(X_SB), .SB_X(SB_X), .S_ADL(S_ADL), .S_S(S_S), .SB_S(SB_S), .S_SB(S_SB),
    .SBx_in(SB_in[5]), .PHI2(PHI2), .ADLx(ADL_out[5]), .Y_Debug(Y_Debug[5]), .X_Debug(X_Debug[5]),
    .S_Debug(S_Debug[5]), .SBx_out(SB_out[5]));
  REGS_BIT r2 (
    .Y_SB(Y_SB), .SB_Y(SB_Y), .X_SB(X_SB), .SB_X(SB_X), .S_ADL(S_ADL), .S_S(S_S), .SB_S(SB_S), .S_SB(S_SB),
    .SBx_in(SB_in[2]), .PHI2(PHI2), .ADLx(ADL_out[2]), .Y_Debug(Y_Debug[2]), .X_Debug(X_Debug[2]),
    .S_Debug(S_Debug[2]), .SBx_out(SB_out[2]));
  REGS_BIT r6 (
    .Y_SB(Y_SB), .SB_Y(SB_Y), .X_SB(X_SB), .SB_X(SB_X), .S_ADL(S_ADL), .S_S(S_S), .SB_S(SB_S), .S_SB(S_SB),
    .SBx_in(SB_in[6]), .PHI2(PHI2), .ADLx(ADL_out[6]), .Y_Debug(Y_Debug[6]), .X_Debug(X_Debug[6]),
    .S_Debug(S_Debug[6]), .SBx_out(SB_out[6]));
  REGS_BIT r3 (
    .Y_SB(Y_SB), .SB_Y(SB_Y), .X_SB(X_SB), .SB_X(SB_X), .S_ADL(S_ADL), .S_S(S_S), .SB_S(SB_S), .S_SB(S_SB),
    .SBx_in(SB_in[3]), .PHI2(PHI2), .ADLx(ADL_out[3]), .Y_Debug(Y_Debug[3]), .X_Debug(X_Debug[3]),
    .S_Debug(S_Debug[3]), .SBx_out(SB_out[3]));
  REGS_BIT r7 (
    .Y_SB(Y_SB), .SB_Y(SB_Y), .X_SB(X_SB), .SB_X(SB_X), .S_ADL(S_ADL), .S_S(S_S), .SB_S(SB_S), .S_SB(S_SB),
    .SBx_in(SB_in[7]), .PHI2(PHI2), .ADLx(ADL_out[7]), .Y_Debug(Y_Debug[7]), .X_Debug(X_Debug[7]),
    .S_Debug(S_Debug[7]), .SBx_out(SB_out[7]));
endmodule

module DL_BIT (
  input  PHI1,
  input  PHI2,
  input  DL_ADL,
  input  DL_ADH,
  input  DL_DB,
  input  RD,
  input  DBx_in,
  input  Dx_in,
  output ADLx,
  output ADHx,
  output DBx_out,
  output Dx_out,
  output DOR_Debug,
  output DL_Debug
);

  wire and_1_out, and_2_out, and_3_out, not_1_out, not_2_out, not_3_out;

  D_Latch DL (.EN(PHI2), .D(not_1_out), .NOT_Q(DL_Debug));  // open: Q
  not not_1 (not_1_out, Dx_in);
  D_Latch DOR (.EN(PHI1), .D(not_2_out), .NOT_Q(DOR_Debug));  // open: Q
  not not_2 (not_2_out, DBx_in);
  and and_1 (and_1_out, DL_ADL, PHI1);
  and and_2 (and_2_out, DL_ADH, PHI1);
  and and_3 (and_3_out, DL_DB, PHI1);
  not not_3 (not_3_out, RD);
  assign ADLx = and_1_out ? DL_Debug : 1'bz;  // Controlled_Buffer controlled_buffer_1
  assign ADHx = and_2_out ? DL_Debug : 1'bz;  // Controlled_Buffer controlled_buffer_2
  assign DBx_out = and_3_out ? DL_Debug : 1'bz;  // Controlled_Buffer controlled_buffer_3
  assign Dx_out = not_3_out ? DOR_Debug : 1'bz;  // Controlled_Buffer controlled_buffer_4
endmodule

module DL (
  input  PHI1,
  input  PHI2,
  input  WR,
  input  DL_ADL,
  input  DL_ADH,
  input  DL_DB,
  input  [7:0] DB_in,
  input  [7:0] Data_in,
  output [7:0] DB_out,
  output [7:0] ADL_out,
  output [7:0] ADH_out,
  output [7:0] Data_out,
  output [7:0] DL_Debug,
  output [7:0] DOR_Debug
);

  wire RD, rd_latch_not_q;

  Multiplexer multiplexer_1 (.in0(rd_latch_not_q), .in1(1'b1), .out(RD), .sel(PHI2));
  D_Latch rd_latch (.EN(PHI1), .D(WR), .NOT_Q(rd_latch_not_q));  // open: Q
  DL_BIT dl0 (
    .DL_ADL(DL_ADL), .DL_ADH(DL_ADH), .DL_DB(DL_DB), .RD(RD), .DBx_in(DB_in[0]), .Dx_in(Data_in[0]),
    .PHI1(PHI1), .PHI2(PHI2), .ADLx(ADL_out[0]), .ADHx(ADH_out[0]), .DBx_out(DB_out[0]),
    .Dx_out(Data_out[0]), .DOR_Debug(DOR_Debug[0]), .DL_Debug(DL_Debug[0]));
  DL_BIT dl1 (
    .DL_ADL(DL_ADL), .DL_ADH(DL_ADH), .DL_DB(DL_DB), .RD(RD), .DBx_in(DB_in[1]), .Dx_in(Data_in[1]),
    .PHI1(PHI1), .PHI2(PHI2), .ADLx(ADL_out[1]), .ADHx(ADH_out[1]), .DBx_out(DB_out[1]),
    .Dx_out(Data_out[1]), .DOR_Debug(DOR_Debug[1]), .DL_Debug(DL_Debug[1]));
  DL_BIT dl2 (
    .DL_ADL(DL_ADL), .DL_ADH(DL_ADH), .DL_DB(DL_DB), .RD(RD), .DBx_in(DB_in[2]), .Dx_in(Data_in[2]),
    .PHI1(PHI1), .PHI2(PHI2), .ADLx(ADL_out[2]), .ADHx(ADH_out[2]), .DBx_out(DB_out[2]),
    .Dx_out(Data_out[2]), .DOR_Debug(DOR_Debug[2]), .DL_Debug(DL_Debug[2]));
  DL_BIT dl3 (
    .DL_ADL(DL_ADL), .DL_ADH(DL_ADH), .DL_DB(DL_DB), .RD(RD), .DBx_in(DB_in[3]), .Dx_in(Data_in[3]),
    .PHI1(PHI1), .PHI2(PHI2), .ADLx(ADL_out[3]), .ADHx(ADH_out[3]), .DBx_out(DB_out[3]),
    .Dx_out(Data_out[3]), .DOR_Debug(DOR_Debug[3]), .DL_Debug(DL_Debug[3]));
  DL_BIT dl4 (
    .DL_ADL(DL_ADL), .DL_ADH(DL_ADH), .DL_DB(DL_DB), .RD(RD), .DBx_in(DB_in[4]), .Dx_in(Data_in[4]),
    .PHI1(PHI1), .PHI2(PHI2), .ADLx(ADL_out[4]), .ADHx(ADH_out[4]), .DBx_out(DB_out[4]),
    .Dx_out(Data_out[4]), .DOR_Debug(DOR_Debug[4]), .DL_Debug(DL_Debug[4]));
  DL_BIT dl5 (
    .DL_ADL(DL_ADL), .DL_ADH(DL_ADH), .DL_DB(DL_DB), .RD(RD), .DBx_in(DB_in[5]), .Dx_in(Data_in[5]),
    .PHI1(PHI1), .PHI2(PHI2), .ADLx(ADL_out[5]), .ADHx(ADH_out[5]), .DBx_out(DB_out[5]),
    .Dx_out(Data_out[5]), .DOR_Debug(DOR_Debug[5]), .DL_Debug(DL_Debug[5]));
  DL_BIT dl6 (
    .DL_ADL(DL_ADL), .DL_ADH(DL_ADH), .DL_DB(DL_DB), .RD(RD), .DBx_in(DB_in[6]), .Dx_in(Data_in[6]),
    .PHI1(PHI1), .PHI2(PHI2), .ADLx(ADL_out[6]), .ADHx(ADH_out[6]), .DBx_out(DB_out[6]),
    .Dx_out(Data_out[6]), .DOR_Debug(DOR_Debug[6]), .DL_Debug(DL_Debug[6]));
  DL_BIT dl7 (
    .DL_ADL(DL_ADL), .DL_ADH(DL_ADH), .DL_DB(DL_DB), .RD(RD), .DBx_in(DB_in[7]), .Dx_in(Data_in[7]),
    .PHI1(PHI1), .PHI2(PHI2), .ADLx(ADL_out[7]), .ADHx(ADH_out[7]), .DBx_out(DB_out[7]),
    .Dx_out(Data_out[7]), .DOR_Debug(DOR_Debug[7]), .DL_Debug(DL_Debug[7]));
endmodule

module ALU (
  input  PHI2,
  input  NDB_ADD,
  input  DB_ADD,
  input  Z_ADD,
  input  SB_ADD,
  input  ADL_ADD,
  input  ADD_SB06,
  input  ADD_SB7,
  input  ADD_ADL,
  input  ANDS,
  input  EORS,
  input  ORS,
  input  SRS,
  input  SUMS,
  input  SB_AC,
  input  AC_SB,
  input  AC_DB,
  input  n_ACIN,
  input  n_DAA,
  input  n_DSA,
  input  [7:0] SB_in,
  input  [7:0] DB_in,
  input  [7:0] ADL_In,
  output ACR,
  output AVR,
  output [7:0] ADD_Debug,
  output [7:0] AC_Debug,
  output [7:0] AI_Debug,
  output [7:0] SB_out,
  output [7:0] BI_Debug,
  output [7:0] DB_out,
  output [7:0] ADL_out
);

  wire ACLatch_q, alu_ops_1_carry4, alu_ops_1_carry6, alu_ops_1_n_carry3, alu_ops_1_n_carry7, and_1_out,
       bcd_carry_1_dc3, bcd_carry_1_dc7, DCLatch_q, nor_1_out, nor_2_out, nor_3_out, not_1_out;
  wire [7:0] alu_add_1_n_addx, alu_bcd_1_out0, alu_ops_1_nand0, alu_ops_1_nor0, alu_ops_1_res0,
       alu_ops_1_xor0;

  ALU_OPS alu_ops_1 (
    .DB_ADD(DB_ADD), .DB5(DB_in[5]), .DB6(DB_in[6]), .DB7(DB_in[7]), .ADL0(ADL_In[0]), .ADL1(ADL_In[1]),
    .ADL2(ADL_In[2]), .ADL3(ADL_In[3]), .ADL4(ADL_In[4]), .ADL5(ADL_In[5]), .Z_ADD(Z_ADD), .ADL6(ADL_In[6]),
    .ADL7(ADL_In[7]), .SB_ADD(SB_ADD), .ADL_ADD(ADL_ADD), .ANDS(ANDS), .EORS(EORS), .ORS(ORS), .SRS(SRS),
    .SUMS(SUMS), .n_cin(n_ACIN), .DC3(bcd_carry_1_dc3), .SB0(SB_in[0]), .SB1(SB_in[1]), .SB2(SB_in[2]),
    .SB3(SB_in[3]), .NDB_ADD(NDB_ADD), .SB4(SB_in[4]), .SB5(SB_in[5]), .SB6(SB_in[6]), .SB7(SB_in[7]),
    .DB0(DB_in[0]), .DB1(DB_in[1]), .DB2(DB_in[2]), .DB3(DB_in[3]), .DB4(DB_in[4]), .BI_Debug(BI_Debug),
    .n_carry3(alu_ops_1_n_carry3), .n_carry7(alu_ops_1_n_carry7), .xor2(alu_ops_1_xor0[2]),
    .xor3(alu_ops_1_xor0[3]), .xor4(alu_ops_1_xor0[4]), .xor5(alu_ops_1_xor0[5]), .xor6(alu_ops_1_xor0[6]),
    .xor7(alu_ops_1_xor0[7]), .res0(alu_ops_1_res0[0]), .res1(alu_ops_1_res0[1]), .res2(alu_ops_1_res0[2]),
    .res3(alu_ops_1_res0[3]), .res4(alu_ops_1_res0[4]), .res5(alu_ops_1_res0[5]), .res6(alu_ops_1_res0[6]),
    .res7(alu_ops_1_res0[7]), .carry4(alu_ops_1_carry4), .nor0(alu_ops_1_nor0[0]), .nor1(alu_ops_1_nor0[1]),
    .nor2(alu_ops_1_nor0[2]), .nor3(alu_ops_1_nor0[3]), .nor4(alu_ops_1_nor0[4]), .nor5(alu_ops_1_nor0[5]),
    .nor6(alu_ops_1_nor0[6]), .nor7(alu_ops_1_nor0[7]), .nand0(alu_ops_1_nand0[0]),
    .carry6(alu_ops_1_carry6), .nand1(alu_ops_1_nand0[1]), .nand2(alu_ops_1_nand0[2]),
    .nand3(alu_ops_1_nand0[3]), .nand4(alu_ops_1_nand0[4]), .nand5(alu_ops_1_nand0[5]),
    .nand6(alu_ops_1_nand0[6]), .nand7(alu_ops_1_nand0[7]), .xor0(alu_ops_1_xor0[0]),
    .xor1(alu_ops_1_xor0[1]), .AI_Debug(AI_Debug));
  BCD_CARRY bcd_carry_1 (
    .n_ACIN(n_ACIN), .carry4(alu_ops_1_carry4), .n_DAA(n_DAA), .nors(alu_ops_1_nor0),
    .nands(alu_ops_1_nand0), .xors(alu_ops_1_xor0), .DC3(bcd_carry_1_dc3), .DC7(bcd_carry_1_dc7));
  nor nor_1 (nor_1_out, alu_ops_1_carry6, alu_ops_1_nand0[7]);
  and and_1 (and_1_out, alu_ops_1_carry6, alu_ops_1_nor0[7]);
  ALU_ADD alu_add_1 (
    .ADD_SB06(ADD_SB06), .ADD_SB7(ADD_SB7), .ADD_ADL(ADD_ADL), .PHI2(PHI2), .n_res(alu_ops_1_res0),
    .n_ADDx(alu_add_1_n_addx), .SB0(SB_out[0]), .SB1(SB_out[1]), .SB2(SB_out[2]), .SB3(SB_out[3]),
    .SB4(SB_out[4]), .SB5(SB_out[5]), .SB6(SB_out[6]), .SB7(SB_out[7]), .ADL0(ADL_out[0]), .ADL1(ADL_out[1]),
    .ADL2(ADL_out[2]), .ADL3(ADL_out[3]), .ADL4(ADL_out[4]), .ADL5(ADL_out[5]), .ADL6(ADL_out[6]),
    .ADL7(ADL_out[7]), .ADD_Debug(ADD_Debug));
  not not_1 (not_1_out, alu_ops_1_n_carry7);
  nor nor_2 (nor_2_out, nor_1_out, and_1_out);
  D_Latch DCLatch (.EN(PHI2), .D(bcd_carry_1_dc7), .Q(DCLatch_q));  // open: NOT_Q
  D_Latch ACLatch (.EN(PHI2), .D(not_1_out), .Q(ACLatch_q));  // open: NOT_Q
  D_Latch AVRLatch (.EN(PHI2), .D(nor_2_out), .NOT_Q(AVR));  // open: Q
  not not_2 (ACR, nor_3_out);
  nor nor_3 (nor_3_out, DCLatch_q, ACLatch_q);
  ALU_BCD alu_bcd_1 (
    .n_carry3(alu_ops_1_n_carry3), .ACR(ACR), .n_DAA(n_DAA), .n_DSA(n_DSA), .SB0(SB_in[0]), .SB1(SB_in[1]),
    .SB2(SB_in[2]), .SB3(SB_in[3]), .SB4(SB_in[4]), .SB5(SB_in[5]), .SB6(SB_in[6]), .PHI2(PHI2),
    .SB7(SB_in[7]), .n_ADDx(alu_add_1_n_addx), .out0(alu_bcd_1_out0[0]), .out1(alu_bcd_1_out0[1]),
    .out2(alu_bcd_1_out0[2]), .out3(alu_bcd_1_out0[3]), .out4(alu_bcd_1_out0[4]), .out5(alu_bcd_1_out0[5]),
    .out6(alu_bcd_1_out0[6]), .out7(alu_bcd_1_out0[7]));
  ALU_AC alu_ac_1 (
    .PHI2(PHI2), .SB_AC(SB_AC), .AC_SB(AC_SB), .AC_DB(AC_DB), .ins(alu_bcd_1_out0), .AC_Debug(AC_Debug),
    .SB_Out(SB_out), .DB_Out(DB_out));

  // Notes on the sheet:
  //   x8
  //   AVR
  //   x8
  //   ACR
  //   x8
endmodule

module PC (
  input  PHI2,
  input  ADL_PCL,
  input  PCL_PCL,
  input  PCL_ADL,
  input  PCL_DB,
  input  ADH_PCH,
  input  PCH_PCH,
  input  PCH_ADH,
  input  PCH_DB,
  input  n_IPC,
  input  [7:0] ADL_in,
  input  [7:0] ADH_in,
  output [7:0] DB,
  output [7:0] ADL_out,
  output [7:0] ADH_out,
  output [15:0] PC_Debug,
  output [15:0] PCS_Debug
);

  wire pcl_1_pclc;

  PCL pcl_1 (
    .cin(n_IPC), .ADL_PCL(ADL_PCL), .PCL_PCL(PCL_PCL), .PCL_ADL(PCL_ADL), .PCL_DB(PCL_DB), .PHI2(PHI2),
    .ADL0(ADL_in[0]), .ADL1(ADL_in[1]), .ADL2(ADL_in[2]), .ADL3(ADL_in[3]), .ADL4(ADL_in[4]),
    .ADL5(ADL_in[5]), .ADL6(ADL_in[6]), .ADL7(ADL_in[7]), .ADL_out0(ADL_out[0]), .ADL_out1(ADL_out[1]),
    .ADL_out2(ADL_out[2]), .ADL_out3(ADL_out[3]), .ADL_out4(ADL_out[4]), .ADL_out5(ADL_out[5]),
    .ADL_out6(ADL_out[6]), .ADL_out7(ADL_out[7]), .DB0(DB[0]), .DB1(DB[1]), .DB2(DB[2]), .DB3(DB[3]),
    .DB4(DB[4]), .DB5(DB[5]), .DB6(DB[6]), .DB7(DB[7]), .PCLS_Debug(PCS_Debug[7:0]),
    .PCL_Debug(PC_Debug[7:0]), .PCLC(pcl_1_pclc));
  PCH pch_1 (
    .cin(pcl_1_pclc), .ADH_PCH(ADH_PCH), .PCH_PCH(PCH_PCH), .PCH_ADH(PCH_ADH), .PCH_DB(PCH_DB), .PHI2(PHI2),
    .ADH0(ADH_in[0]), .ADH1(ADH_in[1]), .ADH2(ADH_in[2]), .ADH3(ADH_in[3]), .ADH4(ADH_in[4]),
    .ADH5(ADH_in[5]), .ADH6(ADH_in[6]), .ADH7(ADH_in[7]), .PCH_Debug(PC_Debug[15:8]),
    .PCHS_Debug(PCS_Debug[15:8]), .ADH_out0(ADH_out[0]), .ADH_out1(ADH_out[1]), .ADH_out2(ADH_out[2]),
    .ADH_out3(ADH_out[3]), .ADH_out4(ADH_out[4]), .ADH_out5(ADH_out[5]), .ADH_out6(ADH_out[6]),
    .ADH_out7(ADH_out[7]), .DB0(DB[0]), .DB1(DB[1]), .DB2(DB[2]), .DB3(DB[3]), .DB4(DB[4]), .DB5(DB[5]),
    .DB6(DB[6]), .DB7(DB[7]));
endmodule

module ABL_BIT (
  input  PHI1,
  input  PHI2,
  input  ADL_ABL,
  input  ADLx,
  output Ax
);

  wire and_1_out, not1_out;

  and and_1 (and_1_out, PHI1, ADL_ABL);
  DFF_Level dff_level_1 (.EN(and_1_out), .D(not1_out), .NOT_Q(Ax));  // open: Q
  not not1 (not1_out, ADLx);

  // Notes on the sheet:
  //   not used
endmodule

module ABH_BIT (
  input  PHI1,
  input  PHI2,
  input  ADH_ABH,
  input  ADHx,
  output Ax
);

  wire and_1_out, not1_out;

  not not1 (not1_out, ADHx);
  and and_1 (and_1_out, PHI1, ADH_ABH);
  DFF_Level dff_level_1 (.EN(and_1_out), .D(not1_out), .NOT_Q(Ax));  // open: Q

  // Notes on the sheet:
  //   not used
endmodule

module PCL_EVEN_BIT (
  input  PHI2,
  input  cin,
  input  ADL_PCL,
  input  PCL_PCL,
  input  PCL_ADL,
  input  PCL_DB,
  input  ADLx_in,
  output DBx,
  output ADLx_out,
  output cout,
  output sout,
  output PCL_Debug,
  output PCLS_Debug
);

  wire and_1_out, controlled_buffer_1_out, nand_1_out, not_1_out, PCL_not_q;

  nor nor_1 (cout, cin, sout);
  nand nand_1 (nand_1_out, cin, sout);
  not not_1 (not_1_out, cout);
  DFF_Posedge PCL (.EN(PHI2), .D(and_1_out), .NOT_Q(PCL_not_q));  // open: Q
  assign controlled_buffer_1_out = PCL_PCL ? PCL_Debug : 1'bz;  // Controlled_Buffer controlled_buffer_1
  assign controlled_buffer_1_out = ADL_PCL ? ADLx_in : 1'bz;  // Controlled_Buffer controlled_buffer_2
  DFF_Level PCLS (.EN(1'b1), .D(controlled_buffer_1_out), .Q(PCLS_Debug), .NOT_Q(sout));
  and and_1 (and_1_out, nand_1_out, not_1_out);
  not not_2 (PCL_Debug, PCL_not_q);
  assign DBx = PCL_DB ? PCL_Debug : 1'bz;  // Controlled_Buffer controlled_buffer_3
  assign ADLx_out = PCL_ADL ? PCL_Debug : 1'bz;  // Controlled_Buffer controlled_buffer_4
endmodule

module PCL_ODD_BIT (
  input  PHI2,
  input  cin,
  input  ADL_PCL,
  input  PCL_PCL,
  input  PCL_ADL,
  input  PCL_DB,
  input  ADLx_in,
  output DBx,
  output ADLx_out,
  output cout,
  output sout,
  output PCL_Debug,
  output PCLS_Debug
);

  wire controlled_buffer_1_out, nor_1_out, not_1_out, not_2_out, not_3_out, or_1_out;

  not not_1 (not_1_out, sout);
  not not_2 (not_2_out, sout);
  nand nand_1 (cout, cin, not_1_out);
  assign controlled_buffer_1_out = PCL_PCL ? PCL_Debug : 1'bz;  // Controlled_Buffer controlled_buffer_1
  assign controlled_buffer_1_out = ADL_PCL ? ADLx_in : 1'bz;  // Controlled_Buffer controlled_buffer_2
  nor nor_1 (nor_1_out, cin, not_2_out);
  or or_1 (or_1_out, nor_1_out, not_3_out);
  not not_3 (not_3_out, cout);
  DFF_Posedge PCL (.EN(PHI2), .D(or_1_out), .NOT_Q(PCL_Debug));  // open: Q
  DFF_Level PCLS (.EN(1'b1), .D(controlled_buffer_1_out), .Q(PCLS_Debug), .NOT_Q(sout));
  assign DBx = PCL_DB ? PCL_Debug : 1'bz;  // Controlled_Buffer controlled_buffer_3
  assign ADLx_out = PCL_ADL ? PCL_Debug : 1'bz;  // Controlled_Buffer controlled_buffer_4
endmodule

module PCH_EVEN_BIT (
  input  PHI2,
  input  cin,
  input  ADH_PCH,
  input  PCH_PCH,
  input  PCH_ADH,
  input  PCH_DB,
  input  ADHx_out,
  output DBx,
  output out_9,
  output cout,
  output sout,
  output PCH_Debug,
  output PCHS_Debug
);

  wire controlled_buffer_1_out, nor_1_out, not_1_out, not_2_out, not_3_out, or_1_out;

  not not_1 (not_1_out, sout);
  not not_2 (not_2_out, sout);
  nand nand_1 (cout, cin, not_1_out);
  assign controlled_buffer_1_out = PCH_PCH ? PCH_Debug : 1'bz;  // Controlled_Buffer controlled_buffer_1
  assign controlled_buffer_1_out = ADH_PCH ? ADHx_out : 1'bz;  // Controlled_Buffer controlled_buffer_2
  nor nor_1 (nor_1_out, cin, not_2_out);
  or or_1 (or_1_out, nor_1_out, not_3_out);
  not not_3 (not_3_out, cout);
  DFF_Posedge PCH (.EN(PHI2), .D(or_1_out), .NOT_Q(PCH_Debug));  // open: Q
  DFF_Level PCHS (.EN(1'b1), .D(controlled_buffer_1_out), .Q(PCHS_Debug), .NOT_Q(sout));
  assign DBx = PCH_DB ? PCH_Debug : 1'bz;  // Controlled_Buffer controlled_buffer_3
  assign out_9 = PCH_ADH ? PCH_Debug : 1'bz;  // Controlled_Buffer controlled_buffer_4
endmodule

module PCH_ODD_BIT (
  input  PHI2,
  input  cin,
  input  ADH_PCH,
  input  PCH_PCH,
  input  PCH_ADH,
  input  PCH_DB,
  input  ADHx_in,
  output DBx,
  output ADHx_out,
  output cout,
  output sout,
  output PCH_Debug,
  output PCHS_Debug
);

  wire and_1_out, controlled_buffer_1_out, nand_1_out, not_1_out, PCH_not_q;

  nor nor_1 (cout, cin, sout);
  nand nand_1 (nand_1_out, cin, sout);
  not not_1 (not_1_out, cout);
  DFF_Posedge PCH (.EN(PHI2), .D(and_1_out), .NOT_Q(PCH_not_q));  // open: Q
  assign controlled_buffer_1_out = PCH_PCH ? PCH_Debug : 1'bz;  // Controlled_Buffer controlled_buffer_1
  assign controlled_buffer_1_out = ADH_PCH ? ADHx_in : 1'bz;  // Controlled_Buffer controlled_buffer_2
  DFF_Level PCHS (.EN(1'b1), .D(controlled_buffer_1_out), .Q(PCHS_Debug), .NOT_Q(sout));
  and and_1 (and_1_out, nand_1_out, not_1_out);
  not not_2 (PCH_Debug, PCH_not_q);
  assign DBx = PCH_DB ? PCH_Debug : 1'bz;  // Controlled_Buffer controlled_buffer_3
  assign ADHx_out = PCH_ADH ? PCH_Debug : 1'bz;  // Controlled_Buffer controlled_buffer_4
endmodule

module PCL (
  input  PHI2,
  input  cin,
  input  ADL_PCL,
  input  PCL_PCL,
  input  PCL_ADL,
  input  PCL_DB,
  input  ADL0,
  input  ADL1,
  input  ADL2,
  input  ADL3,
  input  ADL4,
  input  ADL5,
  input  ADL6,
  input  ADL7,
  output [7:0] PCL_Debug,
  output [7:0] PCLS_Debug,
  output ADL_out0,
  output ADL_out1,
  output ADL_out2,
  output ADL_out3,
  output ADL_out4,
  output ADL_out5,
  output ADL_out6,
  output ADL_out7,
  output DB0,
  output DB1,
  output DB2,
  output DB3,
  output DB4,
  output DB5,
  output DB6,
  output DB7,
  output PCLC
);

  wire pcl0_cout, pcl0_sout, pcl1_cout, pcl1_sout, pcl2_cout, pcl2_sout, pcl3_cout, pcl3_sout, pcl4_cout,
       pcl4_sout, pcl5_cout, pcl5_sout, pcl6_cout, pcl6_sout, pcl7_sout;

  PCL_EVEN_BIT pcl0 (
    .cin(cin), .ADL_PCL(ADL_PCL), .PCL_PCL(PCL_PCL), .PCL_ADL(PCL_ADL), .PCL_DB(PCL_DB), .ADLx_in(ADL0),
    .PHI2(PHI2), .DBx(DB0), .ADLx_out(ADL_out0), .cout(pcl0_cout), .sout(pcl0_sout),
    .PCL_Debug(PCL_Debug[0]), .PCLS_Debug(PCLS_Debug[0]));
  PCL_ODD_BIT pcl1 (
    .cin(pcl0_cout), .ADL_PCL(ADL_PCL), .PCL_PCL(PCL_PCL), .PCL_ADL(PCL_ADL), .PCL_DB(PCL_DB),
    .ADLx_in(ADL1), .PHI2(PHI2), .ADLx_out(ADL_out1), .cout(pcl1_cout), .sout(pcl1_sout),
    .PCL_Debug(PCL_Debug[1]), .PCLS_Debug(PCLS_Debug[1]), .DBx(DB1));
  PCL_EVEN_BIT pcl2 (
    .cin(pcl1_cout), .ADL_PCL(ADL_PCL), .PCL_PCL(PCL_PCL), .PCL_ADL(PCL_ADL), .PCL_DB(PCL_DB),
    .ADLx_in(ADL2), .PHI2(PHI2), .DBx(DB2), .ADLx_out(ADL_out2), .cout(pcl2_cout), .sout(pcl2_sout),
    .PCL_Debug(PCL_Debug[2]), .PCLS_Debug(PCLS_Debug[2]));
  PCL_ODD_BIT pcl3 (
    .cin(pcl2_cout), .ADL_PCL(ADL_PCL), .PCL_PCL(PCL_PCL), .PCL_ADL(PCL_ADL), .PCL_DB(PCL_DB),
    .ADLx_in(ADL3), .PHI2(PHI2), .ADLx_out(ADL_out3), .cout(pcl3_cout), .sout(pcl3_sout),
    .PCL_Debug(PCL_Debug[3]), .PCLS_Debug(PCLS_Debug[3]), .DBx(DB3));
  PCL_EVEN_BIT pcl4 (
    .cin(pcl3_cout), .ADL_PCL(ADL_PCL), .PCL_PCL(PCL_PCL), .PCL_ADL(PCL_ADL), .PCL_DB(PCL_DB),
    .ADLx_in(ADL4), .PHI2(PHI2), .DBx(DB4), .ADLx_out(ADL_out4), .cout(pcl4_cout), .sout(pcl4_sout),
    .PCL_Debug(PCL_Debug[4]), .PCLS_Debug(PCLS_Debug[4]));
  PCL_ODD_BIT pcl5 (
    .cin(pcl4_cout), .ADL_PCL(ADL_PCL), .PCL_PCL(PCL_PCL), .PCL_ADL(PCL_ADL), .PCL_DB(PCL_DB),
    .ADLx_in(ADL5), .PHI2(PHI2), .ADLx_out(ADL_out5), .cout(pcl5_cout), .sout(pcl5_sout),
    .PCL_Debug(PCL_Debug[5]), .PCLS_Debug(PCLS_Debug[5]), .DBx(DB5));
  PCL_EVEN_BIT pcl6 (
    .cin(pcl5_cout), .ADL_PCL(ADL_PCL), .PCL_PCL(PCL_PCL), .PCL_ADL(PCL_ADL), .PCL_DB(PCL_DB),
    .ADLx_in(ADL6), .PHI2(PHI2), .DBx(DB6), .ADLx_out(ADL_out6), .cout(pcl6_cout), .sout(pcl6_sout),
    .PCL_Debug(PCL_Debug[6]), .PCLS_Debug(PCLS_Debug[6]));
  PCL_ODD_BIT pcl7 (
    .cin(pcl6_cout), .ADL_PCL(ADL_PCL), .PCL_PCL(PCL_PCL), .PCL_ADL(PCL_ADL), .PCL_DB(PCL_DB),
    .ADLx_in(ADL7), .PHI2(PHI2), .ADLx_out(ADL_out7), .sout(pcl7_sout), .PCL_Debug(PCL_Debug[7]),
    .PCLS_Debug(PCLS_Debug[7]), .DBx(DB7));  // open: cout
  nor nor_1 (PCLC, pcl0_sout, pcl1_sout, pcl2_sout, pcl3_sout, cin, pcl4_sout, pcl5_sout, pcl6_sout, pcl7_sout);
endmodule

module PCH (
  input  PHI2,
  input  cin,
  input  ADH_PCH,
  input  PCH_PCH,
  input  PCH_ADH,
  input  PCH_DB,
  input  ADH0,
  input  ADH1,
  input  ADH2,
  input  ADH3,
  input  ADH4,
  input  ADH5,
  input  ADH6,
  input  ADH7,
  output ADH_out0,
  output ADH_out1,
  output ADH_out2,
  output ADH_out3,
  output ADH_out4,
  output ADH_out5,
  output ADH_out6,
  output ADH_out7,
  output DB0,
  output DB1,
  output DB2,
  output DB3,
  output DB4,
  output DB5,
  output DB6,
  output DB7,
  output [7:0] PCH_Debug,
  output [7:0] PCHS_Debug
);

  wire nor_1_out, not_1_out, pch0_cout, pch0_sout, pch1_cout, pch1_sout, pch2_cout, pch2_sout, pch3_sout,
       pch4_cout, pch5_cout, pch6_cout;

  not not_1 (not_1_out, cin);
  PCH_EVEN_BIT pch0 (
    .cin(cin), .ADH_PCH(ADH_PCH), .PCH_PCH(PCH_PCH), .PCH_ADH(PCH_ADH), .PCH_DB(PCH_DB), .ADHx_out(ADH0),
    .PHI2(PHI2), .out_9(ADH_out0), .cout(pch0_cout), .sout(pch0_sout), .PCH_Debug(PCH_Debug[0]),
    .PCHS_Debug(PCHS_Debug[0]), .DBx(DB0));
  PCH_ODD_BIT pch1 (
    .cin(pch0_cout), .ADH_PCH(ADH_PCH), .PCH_PCH(PCH_PCH), .PCH_ADH(PCH_ADH), .PCH_DB(PCH_DB),
    .ADHx_in(ADH1), .PHI2(PHI2), .DBx(DB1), .ADHx_out(ADH_out1), .cout(pch1_cout), .sout(pch1_sout),
    .PCH_Debug(PCH_Debug[1]), .PCHS_Debug(PCHS_Debug[1]));
  PCH_EVEN_BIT pch2 (
    .cin(pch1_cout), .ADH_PCH(ADH_PCH), .PCH_PCH(PCH_PCH), .PCH_ADH(PCH_ADH), .PCH_DB(PCH_DB),
    .ADHx_out(ADH2), .PHI2(PHI2), .out_9(ADH_out2), .cout(pch2_cout), .sout(pch2_sout),
    .PCH_Debug(PCH_Debug[2]), .PCHS_Debug(PCHS_Debug[2]), .DBx(DB2));
  PCH_ODD_BIT pch3 (
    .cin(pch2_cout), .ADH_PCH(ADH_PCH), .PCH_PCH(PCH_PCH), .PCH_ADH(PCH_ADH), .PCH_DB(PCH_DB),
    .ADHx_in(ADH3), .PHI2(PHI2), .DBx(DB3), .ADHx_out(ADH_out3), .sout(pch3_sout), .PCH_Debug(PCH_Debug[3]),
    .PCHS_Debug(PCHS_Debug[3]));  // open: cout
  PCH_EVEN_BIT pch4 (
    .cin(nor_1_out), .ADH_PCH(ADH_PCH), .PCH_PCH(PCH_PCH), .PCH_ADH(PCH_ADH), .PCH_DB(PCH_DB),
    .ADHx_out(ADH4), .PHI2(PHI2), .out_9(ADH_out4), .cout(pch4_cout), .PCH_Debug(PCH_Debug[4]),
    .PCHS_Debug(PCHS_Debug[4]), .DBx(DB4));  // open: sout
  PCH_ODD_BIT pch5 (
    .cin(pch4_cout), .ADH_PCH(ADH_PCH), .PCH_PCH(PCH_PCH), .PCH_ADH(PCH_ADH), .PCH_DB(PCH_DB),
    .ADHx_in(ADH5), .PHI2(PHI2), .DBx(DB5), .ADHx_out(ADH_out5), .cout(pch5_cout), .PCH_Debug(PCH_Debug[5]),
    .PCHS_Debug(PCHS_Debug[5]));  // open: sout
  PCH_EVEN_BIT pch6 (
    .cin(pch5_cout), .ADH_PCH(ADH_PCH), .PCH_PCH(PCH_PCH), .PCH_ADH(PCH_ADH), .PCH_DB(PCH_DB),
    .ADHx_out(ADH6), .PHI2(PHI2), .out_9(ADH_out6), .cout(pch6_cout), .PCH_Debug(PCH_Debug[6]),
    .PCHS_Debug(PCHS_Debug[6]), .DBx(DB6));  // open: sout
  PCH_ODD_BIT pch7 (
    .cin(pch6_cout), .ADH_PCH(ADH_PCH), .PCH_PCH(PCH_PCH), .PCH_ADH(PCH_ADH), .PCH_DB(PCH_DB),
    .ADHx_in(ADH7), .PHI2(PHI2), .DBx(DB7), .ADHx_out(ADH_out7), .PCH_Debug(PCH_Debug[7]),
    .PCHS_Debug(PCHS_Debug[7]));  // open: cout, sout
  nor nor_1 (nor_1_out, not_1_out, pch3_sout);

  // Notes on the sheet:
  //   PCHC
endmodule

module ALU_OPS (
  input  NDB_ADD,
  input  DB_ADD,
  input  Z_ADD,
  input  SB_ADD,
  input  ADL_ADD,
  input  ANDS,
  input  EORS,
  input  ORS,
  input  SRS,
  input  SUMS,
  input  n_cin,
  input  DC3,
  input  SB0,
  input  SB1,
  input  SB2,
  input  SB3,
  input  SB4,
  input  SB5,
  input  SB6,
  input  SB7,
  input  DB0,
  input  DB1,
  input  DB2,
  input  DB3,
  input  DB4,
  input  DB5,
  input  DB6,
  input  DB7,
  input  ADL0,
  input  ADL1,
  input  ADL2,
  input  ADL3,
  input  ADL4,
  input  ADL5,
  input  ADL6,
  input  ADL7,
  output n_carry3,
  output carry4,
  output carry6,
  output n_carry7,
  output res0,
  output res1,
  output res2,
  output res3,
  output res4,
  output res5,
  output res6,
  output res7,
  output nor0,
  output nor1,
  output nor2,
  output nor3,
  output nor4,
  output nor5,
  output nor6,
  output nor7,
  output nand0,
  output nand1,
  output nand2,
  output nand3,
  output nand4,
  output nand5,
  output nand6,
  output nand7,
  output xor0,
  output xor1,
  output xor2,
  output xor3,
  output xor4,
  output xor5,
  output xor6,
  output xor7,
  output [7:0] AI_Debug,
  output [7:0] BI_Debug
);

  wire alu0_cout, alu1_n_cout, alu2_cout, alu3_n_cout, alu5_n_cout, not_1_out;

  ALU_EVEN_BIT alu0 (
    .Z_ADD(Z_ADD), .SB_ADD(SB_ADD), .ADL_ADD(ADL_ADD), .ANDS(ANDS), .EORS(EORS), .ORS(ORS), .SRS(SRS),
    .SUMS(SUMS), .n_cin(n_cin), .prev_res(nand1), .SBx(SB0), .NDB_ADD(NDB_ADD), .DBx(DB0), .ADLx(ADL0),
    .DB_ADD(DB_ADD), .AI_Debug(AI_Debug[0]), .BI_Debug(BI_Debug[0]), .n_res(res0), .cout(alu0_cout),
    .r_nor(nor0), .r_nand(nand0), .r_xor(xor0));
  ALU_ODD_BIT alu1 (
    .Z_ADD(Z_ADD), .SB_ADD(SB_ADD), .ADL_ADD(ADL_ADD), .ANDS(ANDS), .EORS(EORS), .ORS(ORS), .SRS(SRS),
    .SUMS(SUMS), .cin(alu0_cout), .prev_res(nand2), .SBx(SB1), .NDB_ADD(NDB_ADD), .DBx(DB1), .ADLx(ADL1),
    .DB_ADD(DB_ADD), .AI_Debug(AI_Debug[1]), .BI_Debug(BI_Debug[1]), .n_res(res1), .n_cout(alu1_n_cout),
    .r_nor(nor1), .r_nand(nand1), .r_xor(xor1));
  ALU_EVEN_BIT alu2 (
    .Z_ADD(Z_ADD), .SB_ADD(SB_ADD), .ADL_ADD(ADL_ADD), .ANDS(ANDS), .EORS(EORS), .ORS(ORS), .SRS(SRS),
    .SUMS(SUMS), .n_cin(alu1_n_cout), .prev_res(nand3), .SBx(SB2), .NDB_ADD(NDB_ADD), .DBx(DB2), .ADLx(ADL2),
    .DB_ADD(DB_ADD), .AI_Debug(AI_Debug[2]), .BI_Debug(BI_Debug[2]), .n_res(res2), .cout(alu2_cout),
    .r_nor(nor2), .r_nand(nand2), .r_xor(xor2));
  ALU_ODD_BIT alu3 (
    .Z_ADD(Z_ADD), .SB_ADD(SB_ADD), .ADL_ADD(ADL_ADD), .ANDS(ANDS), .EORS(EORS), .ORS(ORS), .SRS(SRS),
    .SUMS(SUMS), .cin(alu2_cout), .prev_res(nand4), .SBx(SB3), .NDB_ADD(NDB_ADD), .DBx(DB3), .ADLx(ADL3),
    .DB_ADD(DB_ADD), .AI_Debug(AI_Debug[3]), .BI_Debug(BI_Debug[3]), .n_res(res3), .n_cout(alu3_n_cout),
    .r_nor(nor3), .r_nand(nand3), .r_xor(xor3));
  not not_1 (not_1_out, DC3);
  and and_1 (n_carry3, alu3_n_cout, not_1_out);
  ALU_EVEN_BIT alu4 (
    .Z_ADD(Z_ADD), .SB_ADD(SB_ADD), .ADL_ADD(ADL_ADD), .ANDS(ANDS), .EORS(EORS), .ORS(ORS), .SRS(SRS),
    .SUMS(SUMS), .n_cin(n_carry3), .prev_res(nand5), .SBx(SB4), .NDB_ADD(NDB_ADD), .DBx(DB4), .ADLx(ADL4),
    .DB_ADD(DB_ADD), .AI_Debug(AI_Debug[4]), .BI_Debug(BI_Debug[4]), .n_res(res4), .cout(carry4),
    .r_nor(nor4), .r_nand(nand4), .r_xor(xor4));
  ALU_ODD_BIT alu5 (
    .Z_ADD(Z_ADD), .SB_ADD(SB_ADD), .ADL_ADD(ADL_ADD), .ANDS(ANDS), .EORS(EORS), .ORS(ORS), .SRS(SRS),
    .SUMS(SUMS), .cin(carry4), .prev_res(nand6), .SBx(SB5), .NDB_ADD(NDB_ADD), .DBx(DB5), .ADLx(ADL5),
    .DB_ADD(DB_ADD), .AI_Debug(AI_Debug[5]), .BI_Debug(BI_Debug[5]), .n_res(res5), .n_cout(alu5_n_cout),
    .r_nor(nor5), .r_nand(nand5), .r_xor(xor5));
  ALU_EVEN_BIT alu6 (
    .Z_ADD(Z_ADD), .SB_ADD(SB_ADD), .ADL_ADD(ADL_ADD), .ANDS(ANDS), .EORS(EORS), .ORS(ORS), .SRS(SRS),
    .SUMS(SUMS), .n_cin(alu5_n_cout), .prev_res(nand7), .SBx(SB6), .NDB_ADD(NDB_ADD), .DBx(DB6), .ADLx(ADL6),
    .DB_ADD(DB_ADD), .AI_Debug(AI_Debug[6]), .BI_Debug(BI_Debug[6]), .n_res(res6), .cout(carry6),
    .r_nor(nor6), .r_nand(nand6), .r_xor(xor6));
  ALU_ODD_BIT alu7 (
    .Z_ADD(Z_ADD), .SB_ADD(SB_ADD), .ADL_ADD(ADL_ADD), .ANDS(ANDS), .EORS(EORS), .ORS(ORS), .SRS(SRS),
    .SUMS(SUMS), .cin(carry6), .prev_res(1'b1), .SBx(SB7), .NDB_ADD(NDB_ADD), .DBx(DB7), .ADLx(ADL7),
    .DB_ADD(DB_ADD), .AI_Debug(AI_Debug[7]), .BI_Debug(BI_Debug[7]), .n_res(res7), .n_cout(n_carry7),
    .r_nor(nor7), .r_nand(nand7), .r_xor(xor7));
endmodule

module ALU_EVEN_BIT (
  input  NDB_ADD,
  input  DB_ADD,
  input  Z_ADD,
  input  SB_ADD,
  input  ADL_ADD,
  input  ANDS,
  input  EORS,
  input  ORS,
  input  SRS,
  input  SUMS,
  input  n_cin,
  input  prev_res,
  input  SBx,
  input  DBx,
  input  ADLx,
  output n_res,
  output cout,
  output AI_Debug,
  output r_nor,
  output r_nand,
  output BI_Debug,
  output r_xor
);

  wire and_1_out, controlled_buffer_1_out, controlled_buffer_3_out, nand_2_out, nand_3_out, nand_4_out,
       nor_2_out, not_1_out, not_2_out, not_3_out, not_4_out, not_5_out;

  assign controlled_buffer_1_out = Z_ADD ? 1'b0 : 1'bz;  // Controlled_Buffer controlled_buffer_1
  assign controlled_buffer_1_out = SB_ADD ? SBx : 1'bz;  // Controlled_Buffer controlled_buffer_2
  assign controlled_buffer_3_out = DB_ADD ? DBx : 1'bz;  // Controlled_Buffer controlled_buffer_3
  not not_1 (not_1_out, DBx);
  assign controlled_buffer_3_out = NDB_ADD ? not_1_out : 1'bz;  // Controlled_Buffer controlled_buffer_4
  assign controlled_buffer_3_out = ADL_ADD ? ADLx : 1'bz;  // Controlled_Buffer controlled_buffer_5
  not not_2 (not_2_out, r_nor);
  not not_3 (not_3_out, n_cin);
  D_Latch AI (.EN(1'b1), .D(controlled_buffer_1_out), .Q(AI_Debug));  // open: NOT_Q
  D_Latch BI (.EN(1'b1), .D(controlled_buffer_3_out), .Q(BI_Debug));  // open: NOT_Q
  nand nand_1 (r_nand, AI_Debug, BI_Debug);
  nor nor_1 (r_nor, AI_Debug, BI_Debug);
  nand nand_2 (nand_2_out, not_2_out, r_nand);
  nand nand_3 (nand_3_out, not_3_out, nand_2_out);
  not not_4 (not_4_out, nor_2_out);
  nor nor_2 (nor_2_out, not_3_out, nand_2_out);
  nand nand_4 (nand_4_out, n_cin, r_nand);
  not not_5 (not_5_out, r_nor);
  and and_1 (and_1_out, nand_3_out, not_4_out);
  and and_2 (cout, nand_4_out, not_5_out);
  assign n_res = ANDS ? r_nand : 1'bz;  // Controlled_Buffer controlled_buffer_6
  assign n_res = ORS ? r_nor : 1'bz;  // Controlled_Buffer controlled_buffer_7
  assign n_res = EORS ? nand_2_out : 1'bz;  // Controlled_Buffer controlled_buffer_8
  assign n_res = SRS ? prev_res : 1'bz;  // Controlled_Buffer controlled_buffer_9
  assign n_res = SUMS ? and_1_out : 1'bz;  // Controlled_Buffer controlled_buffer_10
  not not_6 (r_xor, nand_2_out);

  // Notes on the sheet:
  //   xnor
  //   xor
endmodule

module ALU_ODD_BIT (
  input  NDB_ADD,
  input  DB_ADD,
  input  Z_ADD,
  input  SB_ADD,
  input  ADL_ADD,
  input  ANDS,
  input  EORS,
  input  ORS,
  input  SRS,
  input  SUMS,
  input  cin,
  input  prev_res,
  input  SBx,
  input  DBx,
  input  ADLx,
  output n_res,
  output n_cout,
  output AI_Debug,
  output r_nor,
  output r_nand,
  output BI_Debug,
  output r_xor
);

  wire and_1_out, controlled_buffer_1_out, controlled_buffer_3_out, nand_2_out, nand_3_out, nor_3_out,
       not_1_out, not_2_out, not_3_out, not_4_out, not_5_out, not_6_out;

  assign controlled_buffer_1_out = Z_ADD ? 1'b0 : 1'bz;  // Controlled_Buffer controlled_buffer_1
  assign controlled_buffer_1_out = SB_ADD ? SBx : 1'bz;  // Controlled_Buffer controlled_buffer_2
  assign controlled_buffer_3_out = DB_ADD ? DBx : 1'bz;  // Controlled_Buffer controlled_buffer_3
  not not_1 (not_1_out, DBx);
  assign controlled_buffer_3_out = NDB_ADD ? not_1_out : 1'bz;  // Controlled_Buffer controlled_buffer_4
  assign controlled_buffer_3_out = ADL_ADD ? ADLx : 1'bz;  // Controlled_Buffer controlled_buffer_5
  not not_2 (not_2_out, r_nand);
  not not_3 (not_3_out, cin);
  not not_4 (not_4_out, r_nor);
  D_Latch AI (.EN(1'b1), .D(controlled_buffer_1_out), .Q(AI_Debug));  // open: NOT_Q
  D_Latch BI (.EN(1'b1), .D(controlled_buffer_3_out), .Q(BI_Debug));  // open: NOT_Q
  nand nand_1 (r_nand, AI_Debug, BI_Debug);
  nor nor_1 (r_nor, AI_Debug, BI_Debug);
  nor nor_2 (r_xor, not_2_out, r_nor);
  nand nand_2 (nand_2_out, not_3_out, r_xor);
  not not_5 (not_5_out, nor_3_out);
  nor nor_3 (nor_3_out, not_3_out, r_xor);
  nand nand_3 (nand_3_out, cin, not_4_out);
  not not_6 (not_6_out, not_2_out);
  and and_1 (and_1_out, nand_2_out, not_5_out);
  and and_2 (n_cout, nand_3_out, not_6_out);
  assign n_res = ANDS ? r_nand : 1'bz;  // Controlled_Buffer controlled_buffer_6
  assign n_res = ORS ? r_nor : 1'bz;  // Controlled_Buffer controlled_buffer_7
  assign n_res = EORS ? r_xor : 1'bz;  // Controlled_Buffer controlled_buffer_8
  assign n_res = SRS ? prev_res : 1'bz;  // Controlled_Buffer controlled_buffer_9
  assign n_res = SUMS ? and_1_out : 1'bz;  // Controlled_Buffer controlled_buffer_10

  // Notes on the sheet:
  //   xor
  //   xor
endmodule

module BCD_CARRY (
  input  n_ACIN,
  input  carry4,
  input  n_DAA,
  input  [7:0] nors,
  input  [7:0] nands,
  input  [7:0] xors,
  output DC3,
  output DC7
);

  wire and_1_out, nand_1_out, nand_2_out, nor_1_out, nor_2_out, nor_3_out, nor_4_out, nor_5_out, nor_6_out,
       nor_7_out, nor_8_out, nor_9_out, nor_10_out, not_1_out, not_2_out, not_3_out, not_4_out, not_5_out,
       not_6_out, not_7_out, not_8_out, or_1_out, or_2_out;

  and and_1 (and_1_out, n_ACIN, nands[0]);
  not not_1 (not_1_out, nands[5]);
  not not_2 (not_2_out, nands[2]);
  not not_3 (not_3_out, nands[1]);
  nor nor_1 (nor_1_out, and_1_out, nors[0]);
  nor nor_2 (nor_2_out, not_2_out, nors[2]);
  not not_4 (not_4_out, nands[6]);
  nor nor_3 (nor_3_out, not_2_out, xors[3]);
  nor nor_4 (nor_4_out, nor_1_out, nor_2_out, not_3_out, xors[1]);
  not not_5 (not_5_out, nands[1]);
  nand nand_1 (nand_1_out, not_5_out, nor_1_out);
  nor nor_5 (nor_5_out, xors[7], not_4_out);
  nor nor_6 (nor_6_out, carry4, not_1_out, xors[5], xors[6]);
  not not_6 (not_6_out, xors[6]);
  nand nand_2 (nand_2_out, not_1_out, carry4);
  nor nor_7 (nor_7_out, nor_3_out, nor_4_out);
  nor nor_8 (nor_8_out, nors[2], nand_1_out);
  nor nor_9 (nor_9_out, nor_5_out, nor_6_out);
  nor nor_10 (nor_10_out, not_6_out, nand_2_out);
  or or_1 (or_1_out, nor_7_out, nor_8_out);
  not not_7 (not_7_out, n_DAA);
  or or_2 (or_2_out, nor_9_out, nor_10_out);
  not not_8 (not_8_out, n_DAA);
  and and_2 (DC3, or_1_out, not_7_out);
  and and_3 (DC7, or_2_out, not_8_out);

  // Notes on the sheet:
  //   ~/carry4
  //   and5
  //   and5
  //   and1
  //   and1
  //   ~nxor6
  //   b
  //   c
  //   nxor6
  //   ~(b | c)
  //   a
endmodule

module ALU_ADD (
  input  PHI2,
  input  ADD_SB06,
  input  ADD_SB7,
  input  ADD_ADL,
  input  [7:0] n_res,
  output [7:0] n_ADDx,
  output SB0,
  output SB1,
  output SB2,
  output SB3,
  output SB4,
  output SB5,
  output SB6,
  output SB7,
  output ADL0,
  output ADL1,
  output ADL2,
  output ADL3,
  output ADL4,
  output ADL5,
  output ADL6,
  output ADL7,
  output [7:0] ADD_Debug
);

  D_Latch d_latch_1 (.EN(PHI2), .D(n_res[0]), .Q(n_ADDx[0]), .NOT_Q(ADD_Debug[0]));
  D_Latch d_latch_2 (.EN(PHI2), .D(n_res[1]), .Q(n_ADDx[1]), .NOT_Q(ADD_Debug[1]));
  D_Latch d_latch_3 (.EN(PHI2), .D(n_res[2]), .Q(n_ADDx[2]), .NOT_Q(ADD_Debug[2]));
  D_Latch d_latch_4 (.EN(PHI2), .D(n_res[3]), .Q(n_ADDx[3]), .NOT_Q(ADD_Debug[3]));
  D_Latch d_latch_5 (.EN(PHI2), .D(n_res[4]), .Q(n_ADDx[4]), .NOT_Q(ADD_Debug[4]));
  D_Latch d_latch_6 (.EN(PHI2), .D(n_res[5]), .Q(n_ADDx[5]), .NOT_Q(ADD_Debug[5]));
  D_Latch d_latch_7 (.EN(PHI2), .D(n_res[6]), .Q(n_ADDx[6]), .NOT_Q(ADD_Debug[6]));
  D_Latch d_latch_8 (.EN(PHI2), .D(n_res[7]), .Q(n_ADDx[7]), .NOT_Q(ADD_Debug[7]));
  assign SB0 = ADD_SB06 ? ADD_Debug[0] : 1'bz;  // Controlled_Buffer controlled_buffer_1
  assign SB1 = ADD_SB06 ? ADD_Debug[1] : 1'bz;  // Controlled_Buffer controlled_buffer_2
  assign SB2 = ADD_SB06 ? ADD_Debug[2] : 1'bz;  // Controlled_Buffer controlled_buffer_3
  assign SB3 = ADD_SB06 ? ADD_Debug[3] : 1'bz;  // Controlled_Buffer controlled_buffer_4
  assign SB4 = ADD_SB06 ? ADD_Debug[4] : 1'bz;  // Controlled_Buffer controlled_buffer_5
  assign SB5 = ADD_SB06 ? ADD_Debug[5] : 1'bz;  // Controlled_Buffer controlled_buffer_6
  assign SB6 = ADD_SB06 ? ADD_Debug[6] : 1'bz;  // Controlled_Buffer controlled_buffer_7
  assign SB7 = ADD_SB7 ? ADD_Debug[7] : 1'bz;  // Controlled_Buffer controlled_buffer_8
  assign ADL0 = ADD_ADL ? ADD_Debug[0] : 1'bz;  // Controlled_Buffer controlled_buffer_9
  assign ADL1 = ADD_ADL ? ADD_Debug[1] : 1'bz;  // Controlled_Buffer controlled_buffer_10
  assign ADL2 = ADD_ADL ? ADD_Debug[2] : 1'bz;  // Controlled_Buffer controlled_buffer_11
  assign ADL3 = ADD_ADL ? ADD_Debug[3] : 1'bz;  // Controlled_Buffer controlled_buffer_12
  assign ADL4 = ADD_ADL ? ADD_Debug[4] : 1'bz;  // Controlled_Buffer controlled_buffer_13
  assign ADL5 = ADD_ADL ? ADD_Debug[5] : 1'bz;  // Controlled_Buffer controlled_buffer_14
  assign ADL6 = ADD_ADL ? ADD_Debug[6] : 1'bz;  // Controlled_Buffer controlled_buffer_15
  assign ADL7 = ADD_ADL ? ADD_Debug[7] : 1'bz;  // Controlled_Buffer controlled_buffer_16
endmodule

module ALU_BCD (
  input  PHI2,
  input  n_carry3,
  input  ACR,
  input  n_DAA,
  input  n_DSA,
  input  SB0,
  input  SB1,
  input  SB2,
  input  SB3,
  input  SB4,
  input  SB5,
  input  SB6,
  input  SB7,
  input  [7:0] n_ADDx,
  output out0,
  output out1,
  output out2,
  output out3,
  output out4,
  output out5,
  output out6,
  output out7
);

  wire and_1_out, and_2_out, and_3_out, and_4_out, daah_latch_not_q, daal_latch_not_q, dsah_latch_not_q,
       dsal_latch_q, nand_1_out, nand_2_out, nand_3_out, nand_4_out, nand_5_out, nand_6_out, nand_7_out,
       nand_8_out, nand_9_out, nand_10_out, nand_11_out, nor_1_out, nor_2_out, nor_3_out, nor_4_out,
       nor_5_out, nor_6_out, nor_7_out, not_1_out, not_2_out, not_3_out, not_4_out, not_5_out, not_6_out,
       not_7_out, not_8_out, not_9_out, not_10_out;

  not not_1 (not_1_out, n_carry3);
  not not_2 (not_2_out, n_DAA);
  nor nor_1 (nor_1_out, n_ADDx[1], n_ADDx[2]);
  nand nand_1 (nand_1_out, n_ADDx[1], n_ADDx[2]);
  nor nor_2 (nor_2_out, n_ADDx[5], n_ADDx[6]);
  nand nand_2 (nand_2_out, n_ADDx[5], n_ADDx[6]);
  nand nand_3 (nand_3_out, not_2_out, not_1_out);
  nor nor_3 (nor_3_out, not_1_out, n_DSA);
  not not_3 (not_3_out, n_DSA);
  D_Latch daal_latch (.EN(PHI2), .D(nand_3_out), .NOT_Q(daal_latch_not_q));  // open: Q
  not not_4 (not_4_out, ACR);
  D_Latch daah_latch (.EN(PHI2), .D(not_2_out), .NOT_Q(daah_latch_not_q));  // open: Q
  D_Latch dsal_latch (.EN(PHI2), .D(nor_3_out), .Q(dsal_latch_q));  // open: NOT_Q
  D_Latch dsah_latch (.EN(PHI2), .D(not_3_out), .NOT_Q(dsah_latch_not_q));  // open: Q
  nand nand_4 (nand_4_out, n_ADDx[1], daal_latch_not_q);
  and and_1 (and_1_out, nand_4_out, nand_5_out);
  nand nand_5 (nand_5_out, ~n_ADDx[1], dsal_latch_q);  // NAND_Gate
  nand nand_6 (nand_6_out, ~nor_1_out, dsal_latch_q);  // NAND_Gate
  and and_2 (and_2_out, nand_6_out, nand_7_out);
  nand nand_7 (nand_7_out, nand_1_out, daal_latch_not_q);
  nand nand_8 (nand_8_out, n_ADDx[5], nor_4_out);
  and and_3 (and_3_out, nand_8_out, nand_9_out);
  nand nand_9 (nand_9_out, ~n_ADDx[5], nor_5_out);  // NAND_Gate
  nand nand_10 (nand_10_out, ~nor_2_out, nor_5_out);  // NAND_Gate
  and and_4 (and_4_out, nand_10_out, nand_11_out);
  nand nand_11 (nand_11_out, nand_2_out, nor_4_out);
  nor nor_4 (nor_4_out, not_4_out, daah_latch_not_q);
  nor nor_5 (nor_5_out, ACR, dsah_latch_not_q);
  nor nor_6 (nor_6_out, daal_latch_not_q, dsal_latch_q);
  not not_5 (not_5_out, SB1);
  not not_6 (not_6_out, SB2);
  not not_7 (not_7_out, SB3);
  nor nor_7 (nor_7_out, nor_4_out, nor_5_out);
  not not_8 (not_8_out, SB5);
  not not_9 (not_9_out, SB6);
  not not_10 (not_10_out, SB7);
  xor xor_1 (out1, nor_6_out, not_5_out);
  xor xor_2 (out2, and_1_out, not_6_out);
  xor xor_3 (out3, and_2_out, not_7_out);
  xor xor_4 (out5, nor_7_out, not_8_out);
  xor xor_5 (out6, and_3_out, not_9_out);
  xor xor_6 (out7, and_4_out, not_10_out);

  assign out0 = SB0;
  assign out4 = SB4;

  // Notes on the sheet:
  //   DAAL
  //   DAAL
  //   DAAH
  //   DSAL
  //   DSAH
  //   DSAL
  //   DAAH
  //   DSAH
endmodule
module ALU_AC (
  input  PHI2,
  input  SB_AC,
  input  AC_SB,
  input  AC_DB,
  input  [7:0] ins,
  output [7:0] AC_Debug,
  output [7:0] SB_Out,
  output [7:0] DB_Out
);

  wire controlled_buffer_1_out, controlled_buffer_2_out, controlled_buffer_3_out, controlled_buffer_4_out,
       controlled_buffer_5_out, controlled_buffer_6_out, controlled_buffer_7_out, controlled_buffer_8_out;

  assign controlled_buffer_1_out = SB_AC ? ins[0] : 1'bz;  // Controlled_Buffer controlled_buffer_1
  assign controlled_buffer_2_out = SB_AC ? ins[1] : 1'bz;  // Controlled_Buffer controlled_buffer_2
  assign controlled_buffer_3_out = SB_AC ? ins[2] : 1'bz;  // Controlled_Buffer controlled_buffer_3
  assign controlled_buffer_4_out = SB_AC ? ins[3] : 1'bz;  // Controlled_Buffer controlled_buffer_4
  assign controlled_buffer_5_out = SB_AC ? ins[4] : 1'bz;  // Controlled_Buffer controlled_buffer_5
  assign controlled_buffer_6_out = SB_AC ? ins[5] : 1'bz;  // Controlled_Buffer controlled_buffer_6
  assign controlled_buffer_7_out = SB_AC ? ins[6] : 1'bz;  // Controlled_Buffer controlled_buffer_7
  assign controlled_buffer_8_out = SB_AC ? ins[7] : 1'bz;  // Controlled_Buffer controlled_buffer_8
  D_Latch d_latch_1 (.EN(PHI2), .D(controlled_buffer_1_out), .Q(AC_Debug[0]));  // open: NOT_Q
  D_Latch d_latch_2 (.EN(PHI2), .D(controlled_buffer_2_out), .Q(AC_Debug[1]));  // open: NOT_Q
  D_Latch d_latch_3 (.EN(PHI2), .D(controlled_buffer_3_out), .Q(AC_Debug[2]));  // open: NOT_Q
  D_Latch d_latch_4 (.EN(PHI2), .D(controlled_buffer_4_out), .Q(AC_Debug[3]));  // open: NOT_Q
  D_Latch d_latch_5 (.EN(PHI2), .D(controlled_buffer_5_out), .Q(AC_Debug[4]));  // open: NOT_Q
  D_Latch d_latch_6 (.EN(PHI2), .D(controlled_buffer_6_out), .Q(AC_Debug[5]));  // open: NOT_Q
  D_Latch d_latch_7 (.EN(PHI2), .D(controlled_buffer_7_out), .Q(AC_Debug[6]));  // open: NOT_Q
  D_Latch d_latch_8 (.EN(PHI2), .D(controlled_buffer_8_out), .Q(AC_Debug[7]));  // open: NOT_Q
  assign DB_Out = AC_DB ? AC_Debug : 8'bz;  // Controlled_Buffer controlled_buffer_9
  assign SB_Out = AC_SB ? AC_Debug : 8'bz;  // Controlled_Buffer controlled_buffer_10
endmodule

module ADD_SB7_Logic (
  input  PHI1,
  input  PHI2,
  input  n_C_OUT,
  input  n_ready,
  input  SR,
  input  n_ROR,
  output n_ADD_SB7
);

  wire cout_latch_not_q, ff_latch1_not_q, ff_latch2_q, multiplexer_1_out, mux_latch1_q, nor_1_out, not_1_out,
       not_2_out, not_3_out, nready_latch_q, sr_latch1_not_q, sr_latch2_q;

  not not_1 (not_1_out, n_C_OUT);
  D_Latch cout_latch (.EN(PHI2), .D(not_1_out), .NOT_Q(cout_latch_not_q));  // open: Q
  D_Latch nready_latch (.EN(PHI1), .D(n_ready), .Q(nready_latch_q));  // open: NOT_Q
  not not_2 (not_2_out, SR);
  nor nor_1 (nor_1_out, nready_latch_q, not_2_out);
  D_Latch mux_latch1 (.EN(PHI2), .D(nor_1_out), .Q(mux_latch1_q));  // open: NOT_Q
  D_Latch sr_latch1 (.EN(PHI2), .D(SR), .NOT_Q(sr_latch1_not_q));  // open: Q
  D_Latch ff_latch2 (.EN(PHI2), .D(ff_latch1_not_q), .Q(ff_latch2_q));  // open: NOT_Q
  not not_3 (not_3_out, multiplexer_1_out);
  Multiplexer multiplexer_1 (.in0(ff_latch2_q), .in1(cout_latch_not_q), .out(multiplexer_1_out), .sel(mux_latch1_q));
  D_Latch ff_latch1 (.EN(PHI1), .D(not_3_out), .NOT_Q(ff_latch1_not_q));  // open: Q
  D_Latch sr_latch2 (.EN(PHI1), .D(sr_latch1_not_q), .Q(sr_latch2_q));  // open: NOT_Q
  nor nor_2 (n_ADD_SB7, ff_latch1_not_q, sr_latch2_q, n_ROR);

  // Notes on the sheet:
  //   FF
endmodule

module PRECHARGE (
  input  PHI2,
  input  Z_ADD,
  input  SB_ADD,
  input  [7:0] SB_In,
  input  [7:0] DB_In,
  input  [7:0] ADL_In,
  input  [7:0] ADH_In,
  output [7:0] SB_Out,
  output [7:0] DB_Out,
  output [7:0] ADL_Out,
  output [7:0] ADH_Out
);

  wire and_1_out, not_1_out;

  not not_1 (not_1_out, PHI2);
  and and_1 (and_1_out, not_1_out, Z_ADD, SB_ADD);
  Multiplexer #(.width(8)) multiplexer_1 (.in0(SB_In), .in1({8{1'b0}}), .out(SB_Out), .sel(and_1_out));
  Multiplexer #(.width(8)) multiplexer_2 (.in0(DB_In), .in1({8{1'b0}}), .out(DB_Out), .sel(and_1_out));
  Multiplexer #(.width(8)) multiplexer_3 (.in0(ADL_In), .in1({8{1'b0}}), .out(ADL_Out), .sel(and_1_out));
  Multiplexer #(.width(8)) multiplexer_4 (.in0(ADH_In), .in1({8{1'b0}}), .out(ADH_Out), .sel(and_1_out));

  // Notes on the sheet:
  //   SB_In: pull=up
  //   DB_In: pull=up
  //   ADL_In: pull=up
  //   ADH_In: pull=up
  //   Take into account that the tristate bus inputs are pulled up to 1, to simulate precharge.
endmodule

module CONST_GEN (
  input  Z_ADL0,
  input  Z_ADL1,
  input  Z_ADL2,
  input  [7:0] ADL_In,
  input  Z_ADH0,
  input  Z_ADH17,
  input  [7:0] ADH_In,
  output [7:0] ADL_Out,
  output [7:0] ADH_Out
);

  and and_1 (ADL_Out[0], ADL_In[0], ~Z_ADL0);  // AND_Gate
  and and_2 (ADL_Out[1], ADL_In[1], ~Z_ADL1);  // AND_Gate
  and and_3 (ADL_Out[2], ADL_In[2], ~Z_ADL2);  // AND_Gate
  and and_4 (ADH_Out[0], ADH_In[0], ~Z_ADH0);  // AND_Gate
  and and_5 (ADH_Out[1], ADH_In[1], ~Z_ADH17);  // AND_Gate
  and and_6 (ADH_Out[2], ADH_In[2], ~Z_ADH17);  // AND_Gate
  and and_7 (ADH_Out[3], ADH_In[3], ~Z_ADH17);  // AND_Gate
  and and_8 (ADH_Out[4], ADH_In[4], ~Z_ADH17);  // AND_Gate
  and and_9 (ADH_Out[5], ADH_In[5], ~Z_ADH17);  // AND_Gate
  and and_10 (ADH_Out[6], ADH_In[6], ~Z_ADH17);  // AND_Gate
  and and_11 (ADH_Out[7], ADH_In[7], ~Z_ADH17);  // AND_Gate

  assign ADL_Out[7:3] = ADL_In[7:3];
endmodule

module BUS_MUX_HACK (
  input  Y_SB,
  input  X_SB,
  input  S_SB,
  input  AC_DB,
  input  AC_SB,
  input  ADD_SB06,
  input  ADD_SB7,
  input  PCL_DB,
  input  PCH_DB,
  input  PCH_ADH,
  input  DL_ADH,
  input  DL_DB,
  output SB_Dirty,
  output DB_Dirty,
  output ADH_Dirty,
  output SBDB_Clutch
);

  wire or_1_out, or_2_out, or_3_out;

  or or_1 (or_1_out, ADD_SB06, ADD_SB7);
  or or_2 (or_2_out, Y_SB, or_1_out);
  or or_3 (or_3_out, AC_DB, PCL_DB, PCH_DB, DL_DB);
  or or_4 (ADH_Dirty, PCH_ADH, DL_ADH);
  and and_1 (SBDB_Clutch, or_2_out, or_3_out);
  Multiplexer multiplexer_1 (.in0(or_2_out), .in1(1'b0), .out(SB_Dirty), .sel(SBDB_Clutch));
  Multiplexer multiplexer_2 (.in0(or_3_out), .in1(1'b0), .out(DB_Dirty), .sel(SBDB_Clutch));
endmodule

module D_Latch (
  input  EN,
  input  D,
  output Q,
  output NOT_Q
);

  D_Flip_Flop #(.trigger("high")) d_ff_1 (.D(D), .clk(EN), .Q(Q), .Qn(NOT_Q));  // open: preset, reset
endmodule

module DFF_Level (
  input  EN,
  input  D,
  output Q,
  output NOT_Q
);

  D_Flip_Flop #(.trigger("high")) d_ff_1 (.D(D), .clk(EN), .Q(Q), .Qn(NOT_Q));  // open: preset, reset

  // Notes on the sheet:
  //   To simplify importing into Logisim Evo.
endmodule

module DFF_Posedge (
  input  EN,
  input  D,
  output Q,
  output NOT_Q
);

  D_Flip_Flop #(.trigger("falling")) d_ff_1 (.D(D), .clk(EN), .Q(Q), .Qn(NOT_Q));  // open: preset, reset

  // Notes on the sheet:
  //   posedge
  //   To simplify importing into Logisim Evo.
endmodule

module DecoderWithBus (
  input  [5:0] n_TX,
  input  [7:0] IR,
  output [63:0] dec1,
  output [63:0] dec2,
  output IMPL,
  output pp
);

  DECODER_TRANS dec_tran (
    .IR6(IR[6]), .IR5(IR[5]), .n_T0(n_TX[0]), .n_T1X(n_TX[1]), .n_T5(n_TX[5]), .n_T4(n_TX[4]),
    .n_T3(n_TX[3]), .n_T2(n_TX[2]), .IR0(IR[0]), .IR1(IR[1]), .IR7(IR[7]), .IR4(IR[4]), .IR3(IR[3]),
    .IR2(IR[2]), .x10(dec1[10]), .x11(dec1[11]), .x12(dec1[12]), .x13(dec1[13]), .x14(dec1[14]),
    .x15(dec1[15]), .x16(dec1[16]), .x17(dec1[17]), .x18(dec1[18]), .x19(dec1[19]), .x20(dec1[20]),
    .x21(dec1[21]), .x22(dec1[22]), .x23(dec1[23]), .x24(dec1[24]), .x25(dec1[25]), .x26(dec1[26]),
    .x27(dec1[27]), .x28(dec1[28]), .x29(dec1[29]), .x30(dec1[30]), .x31(dec1[31]), .x32(dec1[32]),
    .x33(dec1[33]), .x34(dec1[34]), .x35(dec1[35]), .x36(dec1[36]), .x37(dec1[37]), .x38(dec1[38]),
    .x39(dec1[39]), .x40(dec1[40]), .x41(dec1[41]), .x42(dec1[42]), .x43(dec1[43]), .x44(dec1[44]),
    .x0(dec1[0]), .x45(dec1[45]), .x46(dec1[46]), .x47(dec1[47]), .x48(dec1[48]), .x49(dec1[49]),
    .x50(dec1[50]), .x51(dec1[51]), .x52(dec1[52]), .x53(dec1[53]), .x1(dec1[1]), .x54(dec1[54]),
    .x55(dec1[55]), .x56(dec1[56]), .x57(dec1[57]), .x58(dec1[58]), .x59(dec1[59]), .x60(dec1[60]),
    .x61(dec1[61]), .x62(dec1[62]), .x2(dec1[2]), .x63(dec1[63]), .x64(dec2[0]), .x65(dec2[1]),
    .x66(dec2[2]), .x67(dec2[3]), .x68(dec2[4]), .x69(dec2[5]), .x70(dec2[6]), .x71(dec2[7]), .x72(dec2[8]),
    .x3(dec1[3]), .x73(dec2[9]), .x74(dec2[10]), .x75(dec2[11]), .x76(dec2[12]), .x77(dec2[13]),
    .x78(dec2[14]), .x79(dec2[15]), .x80(dec2[16]), .x81(dec2[17]), .x4(dec1[4]), .x82(dec2[18]),
    .x83(dec2[19]), .x84(dec2[20]), .x85(dec2[21]), .x86(dec2[22]), .x87(dec2[23]), .x88(dec2[24]),
    .x89(dec2[25]), .x90(dec2[26]), .x5(dec1[5]), .x91(dec2[27]), .x92(dec2[28]), .x93(dec2[29]),
    .x94(dec2[30]), .x95(dec2[31]), .x96(dec2[32]), .x97(dec2[33]), .x98(dec2[34]), .x99(dec2[35]),
    .x100(dec2[36]), .x101(dec2[37]), .x102(dec2[38]), .x103(dec2[39]), .x104(dec2[40]), .x105(dec2[41]),
    .x106(dec2[42]), .x107(dec2[43]), .x108(dec2[44]), .x109(dec2[45]), .x6(dec1[6]), .x110(dec2[46]),
    .x111(dec2[47]), .x112(dec2[48]), .x113(dec2[49]), .x114(dec2[50]), .x115(dec2[51]), .x116(dec2[52]),
    .x117(dec2[53]), .x118(dec2[54]), .x119(dec2[55]), .x7(dec1[7]), .x120(dec2[56]), .x121(dec2[57]),
    .x122(dec2[58]), .x123(dec2[59]), .x124(dec2[60]), .x125(dec2[61]), .x126(dec2[62]), .x127(dec2[63]),
    .x128(IMPL), .x129(pp), .x8(dec1[8]), .x9(dec1[9]));
endmodule

module TopPart (
);

  // DecoderWithBus decoder: pin names not known
  // DispatchUnit disp: pin names not known
endmodule

module DispatchUnit (
  input  PHI1,
  input  PHI2,
  input  RDY,
  input  PC_DB,
  input  DORES,
  input  RESP,
  input  BRFW,
  input  n_BRTAKEN,
  input  ACR,
  input  n_IMPLIED,
  input  n_TWOCYCLE,
  input  B_OUT,
  input  n_ADL_PCL,
  input  BRK6E,
  input  [63:0] dec2,
  output n_ready,
  output WR,
  output T0,
  output T1,
  output n_T0,
  output n_T1X,
  output T6,
  output T7,
  output ACRL2,
  output TRES2,
  output n_IPC,
  output STOR,
  output Z_IR,
  output FETCH
);

  wire acrl_acrl1, comp_ends, comp_n_tresx, incpc_bra, n_MemOP, n_SHIFT, not_1_out, ready_rw_notreadyphi1,
       REST;

  not not_1 (not_1_out, dec2[33]);
  nor nor_1 (n_SHIFT, dec2[42], dec2[43]);
  nor nor_2 (n_MemOP, dec2[47], dec2[58], dec2[59], dec2[60], dec2[61]);
  nand nand_1 (REST, n_SHIFT, not_1_out);
  nor nor_3 (STOR, n_MemOP, not_1_out);
  DispReadyRW ready_rw (
    .PHI1(PHI1), .PHI2(PHI2), .RDY(RDY), .STOR(STOR), .PC_DB(PC_DB), .D98(dec2[34]), .D100(dec2[36]),
    .T6(T6), .T7(T7), .DORES(DORES), .n_ready(n_ready), .NotReadyPhi1(ready_rw_notreadyphi1), .WR(WR));
  DispACRLatch acrl (
    .PHI1(PHI1), .PHI2(PHI2), .ACR(ACR), .NotReadyPhi1(ready_rw_notreadyphi1), .ACRL1(acrl_acrl1),
    .ACRL2(ACRL2));
  DispRMWCycle rmw (
    .PHI1(PHI1), .PHI2(PHI2), .n_ready(n_ready), .n_SHIFT(n_SHIFT), .n_MemOP(n_MemOP), .T6(T6), .T7(T7));
  DispShortCycle short (
    .PHI1(PHI1), .PHI2(PHI2), .n_ready(n_ready), .RESP(RESP), .BRA(incpc_bra), .ENDS(comp_ends),
    .n_TWOCYCLE(n_TWOCYCLE), .n_TRESX(comp_n_tresx), .T1(T1), .n_T0(n_T0), .T0(T0), .n_T1X(n_T1X));
  DispCompletionUnit comp (
    .PHI1(PHI1), .PHI2(PHI2), .n_ready(n_ready), .ACRL1(acrl_acrl1), .D91(dec2[27]), .D92(dec2[28]),
    .REST(REST), .BRK6E(BRK6E), .RESP(RESP), .n_SHIFT(n_SHIFT), .n_MemOP(n_MemOP), .T7(T7), .D96(dec2[32]),
    .D100(dec2[36]), .D101(dec2[37]), .D102(dec2[38]), .D103(dec2[39]), .D104(dec2[40]), .D105(dec2[41]),
    .T0(T0), .n_BRTAKEN(n_BRTAKEN), .T1(T1), .BR2(dec2[16]), .BR3(dec2[29]), .TRES2(TRES2),
    .n_TRESX(comp_n_tresx), .ENDS(comp_ends));
  DispIncrementPC incpc (
    .PHI1(PHI1), .PHI2(PHI2), .B_OUT(B_OUT), .NotReadyPhi1(ready_rw_notreadyphi1), .BRFW(BRFW), .ACR(ACR),
    .n_ready(n_ready), .n_BRTAKEN(n_BRTAKEN), .n_ADL_PCL(n_ADL_PCL), .n_IMPLIED(n_IMPLIED), .BR2(dec2[16]),
    .BR3(dec2[29]), .BRA(incpc_bra), .n_IPC(n_IPC));
  DispFetch fetch_unit (.B_OUT(B_OUT), .PHI2(PHI2), .T1(T1), .n_ready(n_ready), .Z_IR(Z_IR), .FETCH(FETCH));

  // Other names for the same wires on the sheet: BR2 = dec2[16]; BR3 = dec2[29]

  // Notes on the sheet:
  //   /STORE
endmodule

module DispReadyRW (
  input  PHI1,
  input  PHI2,
  input  RDY,
  input  STOR,
  input  PC_DB,
  input  D98,
  input  D100,
  input  T6,
  input  T7,
  input  DORES,
  output n_ready,
  output NotReadyPhi1,
  output WR
);

  wire nor_1_out, nor_2_out, rdydelay_latch1_not_q, ready_latch1_not_q, ready_latch2_q, wr_latch_q;

  nor nor_1 (nor_1_out, STOR, PC_DB, D98, D100, T6, T7);
  D_Latch wr_latch (.EN(PHI2), .D(nor_1_out), .Q(wr_latch_q));  // open: NOT_Q
  nor nor_2 (nor_2_out, RDY, ready_latch2_q);
  nor nor_3 (WR, n_ready, wr_latch_q, DORES);
  D_Latch ready_latch1 (.EN(PHI2), .D(nor_2_out), .NOT_Q(ready_latch1_not_q));  // open: Q
  D_Latch ready_latch2 (.EN(PHI1), .D(WR), .Q(ready_latch2_q));  // open: NOT_Q
  not not_1 (n_ready, ready_latch1_not_q);
  D_Latch rdydelay_latch1 (.EN(PHI1), .D(n_ready), .NOT_Q(rdydelay_latch1_not_q));  // open: Q
  D_Latch rdydelay_latch2 (.EN(PHI2), .D(rdydelay_latch1_not_q), .NOT_Q(NotReadyPhi1));  // open: Q

  // Notes on the sheet:
  //   RDY
  //   RDY_FF
  //   ReadyDelay
endmodule

module DispShortCycle (
  input  PHI1,
  input  PHI2,
  input  n_ready,
  input  RESP,
  input  BRA,
  input  ENDS,
  input  n_TWOCYCLE,
  input  n_TRESX,
  output T1,
  output n_T0,
  output T0,
  output n_T1X
);

  wire and_1_out, comp_latch1_q, comp_latch2_q, comp_latch3_q, nor_1_out, nor_2_out, nor_3_out, nor_4_out,
       nor_5_out, nor_6_out, nor_8_out, not_1_out, not_2_out, nready_latch_q, step_latch1_q, step_latch2_q,
       t0_latch_q, t1x_latch_q;

  D_Latch nready_latch (.EN(PHI1), .D(not_1_out), .Q(nready_latch_q));  // open: NOT_Q
  not not_1 (not_1_out, n_ready);
  D_Latch comp_latch1 (.EN(PHI1), .D(not_2_out), .Q(comp_latch1_q));  // open: NOT_Q
  D_Latch comp_latch2 (.EN(PHI1), .D(n_TWOCYCLE), .Q(comp_latch2_q));  // open: NOT_Q
  D_Latch comp_latch3 (.EN(PHI1), .D(n_TRESX), .Q(comp_latch3_q));  // open: NOT_Q
  and and_1 (and_1_out, comp_latch2_q, comp_latch3_q);
  nor nor_1 (nor_1_out, comp_latch1_q, and_1_out);
  nor nor_2 (nor_2_out, t0_latch_q, t1x_latch_q);
  nor nor_3 (nor_3_out, RESP, nready_latch_q, step_latch2_q);
  nor nor_4 (nor_4_out, step_latch1_q, BRA);
  nor nor_5 (nor_5_out, nor_4_out, n_ready);
  nor nor_6 (nor_6_out, nor_5_out, ENDS);
  nor nor_7 (n_T0, nor_1_out, nor_2_out);
  nor nor_8 (nor_8_out, t0_latch_q, n_ready);
  D_Latch step_latch1 (.EN(PHI2), .D(nor_3_out), .Q(step_latch1_q));  // open: NOT_Q
  D_Latch step_latch2 (.EN(PHI1), .D(nor_4_out), .Q(step_latch2_q));  // open: NOT_Q
  D_Latch t1_latch (.EN(PHI1), .D(nor_6_out), .NOT_Q(T1));  // open: Q
  not not_2 (not_2_out, nor_6_out);
  D_Latch t0_latch (.EN(PHI2), .D(n_T0), .Q(t0_latch_q));  // open: NOT_Q
  D_Latch t1x_latch (.EN(PHI1), .D(nor_8_out), .Q(t1x_latch_q), .NOT_Q(n_T1X));
  not not_3 (T0, n_T0);

  // Notes on the sheet:
  //   ENDS
  //   STEP_FF
  //   T0_FF
  //   TRES1
endmodule

module DispRMWCycle (
  input  PHI1,
  input  PHI2,
  input  n_ready,
  input  n_SHIFT,
  input  n_MemOP,
  output T6,
  output T7
);

  wire and_1_out, nand_1_out, nor_1_out, nor_2_out, not_1_out, t6_latch2_q, t7_latch1_not_q, t7_latch2_not_q,
       t67_latch_q;

  nor nor_1 (nor_1_out, n_SHIFT, n_MemOP, n_ready);
  and and_1 (and_1_out, t6_latch2_q, n_ready);
  D_Latch t67_latch (.EN(PHI2), .D(nor_1_out), .Q(t67_latch_q));  // open: NOT_Q
  nor nor_2 (nor_2_out, and_1_out, t67_latch_q);
  D_Latch t6_latch2 (.EN(PHI2), .D(T6), .Q(t6_latch2_q));  // open: NOT_Q
  D_Latch t6_latch1 (.EN(PHI1), .D(nor_2_out), .NOT_Q(T6));  // open: Q
  not not_1 (not_1_out, n_ready);
  nand nand_1 (nand_1_out, T6, not_1_out);
  D_Latch t7_latch1 (.EN(PHI2), .D(nand_1_out), .NOT_Q(t7_latch1_not_q));  // open: Q
  D_Latch t7_latch2 (.EN(PHI1), .D(t7_latch1_not_q), .NOT_Q(t7_latch2_not_q));  // open: Q
  not not_2 (T7, t7_latch2_not_q);

  // Notes on the sheet:
  //   T6_FF
endmodule

module DispCompletionUnit (
  input  PHI1,
  input  PHI2,
  input  n_ready,
  input  ACRL1,
  input  D91,
  input  D92,
  input  REST,
  input  BRK6E,
  input  RESP,
  input  n_SHIFT,
  input  n_MemOP,
  input  T7,
  input  D96,
  input  D100,
  input  D101,
  input  D102,
  input  D103,
  input  D104,
  input  D105,
  input  T0,
  input  n_BRTAKEN,
  input  T1,
  input  BR2,
  input  BR3,
  output TRES2,
  output n_TRESX,
  output ENDS
);

  wire and_1_out, ends_latch1_q, ends_latch2_q, multiplexer_1_out, nor_1_out, nor_2_out, nor_3_out,
       nor_4_out, nor_6_out, nor_7_out, nor_8_out, nor_9_out, not_1_out, not_2_out, not_3_out,
       tresx_latch1_q, tresx_latch2_not_q;

  nor nor_1 (nor_1_out, D91, D92);
  nor nor_2 (nor_2_out, D100, D101, D102, D103, D104, D105);
  not not_1 (not_1_out, nor_2_out);
  and and_1 (and_1_out, n_BRTAKEN, BR2);
  nor nor_3 (nor_3_out, T0, and_1_out);
  not not_2 (not_2_out, T1);
  Multiplexer multiplexer_1 (.in0(nor_3_out), .in1(not_2_out), .out(multiplexer_1_out), .sel(n_ready));
  D_Latch tresx_latch1 (.EN(PHI2), .D(nor_1_out), .Q(tresx_latch1_q));  // open: NOT_Q
  not not_3 (not_3_out, n_SHIFT);
  nor nor_4 (nor_4_out, D96, not_3_out, n_MemOP);
  D_Latch ends_latch1 (.EN(PHI2), .D(multiplexer_1_out), .Q(ends_latch1_q));  // open: NOT_Q
  D_Latch ends_latch2 (.EN(PHI2), .D(RESP), .Q(ends_latch2_q));  // open: NOT_Q
  nor nor_5 (ENDS, ends_latch1_q, ends_latch2_q);
  nor nor_6 (nor_6_out, nor_4_out, T7, not_1_out, BR3);
  nor nor_7 (nor_7_out, ACRL1, tresx_latch1_q, n_ready, REST);
  nor nor_8 (nor_8_out, RESP, ENDS, nor_9_out);
  nor nor_9 (nor_9_out, n_ready, nor_6_out);
  nor nor_10 (n_TRESX, nor_7_out, BRK6E, tresx_latch2_not_q);
  D_Latch tres2_latch (.EN(PHI1), .D(n_TRESX), .NOT_Q(TRES2));  // open: Q
  D_Latch tresx_latch2 (.EN(PHI2), .D(nor_8_out), .NOT_Q(tresx_latch2_not_q));  // open: Q

  // Notes on the sheet:
  //   ENDS
  //   ENDX
endmodule

module DispACRLatch (
  input  PHI1,
  input  PHI2,
  input  ACR,
  input  NotReadyPhi1,
  output ACRL1,
  output ACRL2
);

  wire acr_latch1_not_q, and_1_out, nor_2_out, not_1_out, not_2_out;

  not not_1 (not_1_out, NotReadyPhi1);
  not not_2 (not_2_out, ACR);
  and and_1 (and_1_out, not_2_out, not_1_out);
  nor nor_1 (ACRL1, and_1_out, nor_2_out);
  nor nor_2 (nor_2_out, not_1_out, ACRL2);
  D_Latch acr_latch1 (.EN(PHI1), .D(ACRL1), .NOT_Q(acr_latch1_not_q));  // open: Q
  D_Latch acr_latch2 (.EN(PHI2), .D(acr_latch1_not_q), .NOT_Q(ACRL2));  // open: Q

  // Notes on the sheet:
  //   ACRL_FF
endmodule

module DispIncrementPC (
  input  PHI1,
  input  PHI2,
  input  B_OUT,
  input  NotReadyPhi1,
  input  BRFW,
  input  ACR,
  input  n_ready,
  input  n_BRTAKEN,
  input  n_ADL_PCL,
  input  n_IMPLIED,
  input  BR2,
  input  BR3,
  output BRA,
  output n_IPC
);

  wire and_1_out, br_latch1_q, br_latch2_not_q, ipc_latch1_q, ipc_latch2_q, ipc_latch3_q, nor_1_out,
       nor_2_out, nor_3_out, nor_4_out, nor_5_out, not_1_out, not_2_out, not_3_out, not_4_out, or_1_out,
       xor_1_out;

  not not_1 (not_1_out, n_IMPLIED);
  nor nor_1 (nor_1_out, BR2, BR3);
  not not_2 (not_2_out, nor_1_out);
  and and_1 (and_1_out, n_BRTAKEN, BR2);
  nor nor_2 (nor_2_out, n_ADL_PCL, not_2_out);
  not not_3 (not_3_out, BR3);
  nor nor_3 (nor_3_out, and_1_out, nor_2_out);
  nor nor_4 (nor_4_out, not_3_out, NotReadyPhi1);
  not not_4 (not_4_out, ACR);
  D_Latch br_latch2 (.EN(PHI2), .D(nor_4_out), .NOT_Q(br_latch2_not_q));  // open: Q
  xor xor_1 (xor_1_out, BRFW, not_4_out);
  D_Latch br_latch1 (.EN(PHI2), .D(nor_3_out), .Q(br_latch1_q));  // open: NOT_Q
  and and_2 (BRA, ~br_latch2_not_q, xor_1_out);  // AND_Gate
  nor nor_5 (nor_5_out, n_ready, br_latch1_q, not_1_out);
  D_Latch ipc_latch1 (.EN(PHI1), .D(B_OUT), .Q(ipc_latch1_q));  // open: NOT_Q
  D_Latch ipc_latch2 (.EN(PHI1), .D(BRA), .Q(ipc_latch2_q));  // open: NOT_Q
  D_Latch ipc_latch3 (.EN(PHI1), .D(nor_5_out), .Q(ipc_latch3_q));  // open: NOT_Q
  or or_1 (or_1_out, ipc_latch2_q, ipc_latch3_q);
  nand nand_1 (n_IPC, ipc_latch1_q, or_1_out);

  // Notes on the sheet:
  //   Branch 2
  //   Branch 3
  //   Branch 1
  //   Crazy combo (check out tran!)
endmodule

module DispFetch (
  input  B_OUT,
  input  PHI2,
  input  T1,
  input  n_ready,
  output Z_IR,
  output FETCH
);

  wire fetch_latch_not_q;

  D_Latch fetch_latch (.EN(PHI2), .D(T1), .NOT_Q(fetch_latch_not_q));  // open: Q
  nor nor_1 (FETCH, fetch_latch_not_q, n_ready);
  nand nand_1 (Z_IR, B_OUT, FETCH);
endmodule

module INT_FF (
  input  phi2,
  input  d,
  output q,
  output nq
);

  wire and_1_out, and_2_out, not_1_out;

  not not_1 (not_1_out, d);
  and and_1 (and_1_out, phi2, not_1_out);
  nor nor_1 (q, and_1_out, nq);
  and and_2 (and_2_out, phi2, d);
  nor nor_2 (nq, and_2_out, q);

  // Notes on the sheet:
  //   phi2=1: enable
  //   aoi21 flip-flop
endmodule

module BotPart (
  input  PHI1,
  input  PHI2,
  input  WR,
  input  [43:0] bop,
  input  n_ACIN,
  input  n_DAA,
  input  n_DSA,
  input  n_IPC,
  input  [7:0] DB_in,
  input  [7:0] DataBus_in,
  output [15:0] A,
  output [7:0] DB_out,
  output [7:0] DataBus_out,
  output ACR,
  output AVR
);

  wire [7:0] busmux_inst_adh_out, busmux_inst_adl_out, busmux_inst_sb_out, pc_inst_adh_out,
       regs_inst_adl_out, regs_inst_s_debug, regs_inst_sb_out, regs_inst_x_debug, regs_inst_y_debug;
  wire [15:0] pc_inst_pc_debug, pc_inst_pcs_debug;

  ABL ablo (.ADL(busmux_inst_adl_out), .PHI1(PHI1), .PHI2(PHI2), .ADL_ABL(bop[33]), .A(A[7:0]));
  ABH abhi (.ADH(busmux_inst_adh_out), .PHI2(PHI2), .ADH_ABH(bop[32]), .PHI1(PHI1), .A(A[15:8]));
  REGS regs_inst (
    .SB_in(busmux_inst_sb_out), .PHI2(PHI2), .Y_SB(bop[0]), .SB_Y(bop[1]), .X_SB(bop[2]), .SB_X(bop[3]),
    .S_ADL(bop[4]), .S_S(bop[7]), .SB_S(bop[6]), .S_SB(bop[5]), .S_Debug(regs_inst_s_debug),
    .SB_out(regs_inst_sb_out), .ADL_out(regs_inst_adl_out), .Y_Debug(regs_inst_y_debug),
    .X_Debug(regs_inst_x_debug));
  // Probe on regs_inst_s_debug
  // Probe on regs_inst_y_debug
  // Probe on regs_inst_x_debug
  // Probe on busmux_inst_sb_out
  BusMux busmux_inst (
    .PHI2(PHI2), .bop(bop), .SB_in(regs_inst_sb_out), .DB_in(DB_in), .ADL_in(regs_inst_adl_out),
    .ADH_in(pc_inst_adh_out), .SB_out(busmux_inst_sb_out), .DB_out(DB_out), .ADL_out(busmux_inst_adl_out),
    .ADH_out(busmux_inst_adh_out));
  // Probe on regs_inst_sb_out
  // Probe on DB_in
  // Probe on regs_inst_adl_out
  ALU alu_inst (
    .NDB_ADD(bop[8]), .DB_ADD(bop[9]), .Z_ADD(bop[10]), .SB_ADD(bop[11]), .ADL_ADD(bop[12]),
    .ADD_SB06(bop[19]), .ADD_SB7(bop[18]), .ADD_ADL(bop[20]), .ANDS(bop[13]), .EORS(bop[14]), .ORS(bop[15]),
    .SRS(bop[16]), .PHI2(PHI2), .SUMS(bop[17]), .SB_AC(bop[21]), .AC_SB(bop[22]), .AC_DB(bop[23]),
    .n_ACIN(n_ACIN), .n_DAA(n_DAA), .n_DSA(n_DSA), .ADL_In(busmux_inst_adl_out), .SB_in(busmux_inst_sb_out),
    .DB_in(DB_out), .ACR(ACR), .AVR(AVR), .SB_out(regs_inst_sb_out), .DB_out(DB_in),
    .ADL_out(regs_inst_adl_out));  // open: AC_Debug, AI_Debug, BI_Debug, ADD_Debug
  // Probe on busmux_inst_adl_out
  // Probe on busmux_inst_adh_out
  PC pc_inst (
    .ADL_PCL(bop[28]), .PCL_PCL(bop[29]), .PCL_ADL(bop[30]), .PCL_DB(bop[31]), .ADH_PCH(bop[24]),
    .PCH_PCH(bop[25]), .PCH_ADH(bop[26]), .PCH_DB(bop[27]), .n_IPC(n_IPC), .PHI2(PHI2),
    .ADL_in(busmux_inst_adl_out), .ADH_in(busmux_inst_adh_out), .DB(DB_in), .ADL_out(regs_inst_adl_out),
    .ADH_out(pc_inst_adh_out), .PC_Debug(pc_inst_pc_debug), .PCS_Debug(pc_inst_pcs_debug));
  // Probe on pc_inst_pc_debug
  // Probe on pc_inst_pcs_debug
  // Probe on regs_inst_adl_out
  // Probe on pc_inst_adh_out
  DL dl_inst (
    .DB_in(DB_out), .Data_in(DataBus_in), .PHI1(PHI1), .PHI2(PHI2), .WR(WR), .DL_ADL(bop[41]),
    .DL_ADH(bop[42]), .DL_DB(bop[43]), .DB_out(DB_in), .ADL_out(regs_inst_adl_out),
    .ADH_out(pc_inst_adh_out), .Data_out(DataBus_out));  // open: DOR_Debug, DL_Debug
  // Probe on DB_out

  // Other names for the same wires on the sheet: Y_SB = bop[0]; SB_Y = bop[1]; X_SB = bop[2]; SB_X = bop[3];
  //   S_ADL = bop[4]; S_SB = bop[5]; SB_S = bop[6]; S_S = bop[7]; NDB_ADD = bop[8]; DB_ADD = bop[9]; Z_ADD = bop[10];
  //   SB_ADD = bop[11]; ADL_ADD = bop[12]; ANDS = bop[13]; EORS = bop[14]; ORS = bop[15]; SRS = bop[16];
  //   SUMS = bop[17]; ADD_SB7 = bop[18]; ADD_SB06 = bop[19]; ADD_ADL = bop[20]; SB_AC = bop[21]; AC_SB = bop[22];
  //   AC_DB = bop[23]; ADH_PCH = bop[24]; PCH_PCH = bop[25]; PCH_ADH = bop[26]; PCH_DB = bop[27]; ADL_PCL = bop[28];
  //   PCL_PCL = bop[29]; PCL_ADL = bop[30]; PCL_DB = bop[31]; ADH_ABH = bop[32]; ADL_ABL = bop[33]; Z_ADL0 = bop[34];
  //   Z_ADL1 = bop[35]; Z_ADL2 = bop[36]; Z_ADH0 = bop[37]; Z_ADH17 = bop[38]; SB_DB = bop[39]; SB_ADH = bop[40];
  //   DL_ADL = bop[41]; DL_ADH = bop[42]; DL_DB = bop[43]

  // Notes on the sheet:
  //   external databus
  //   from flags
  //   external databus
  //   to flags
endmodule

module BusMux (
  input  PHI2,
  input  [43:0] bop,
  input  [7:0] SB_in,
  input  [7:0] DB_in,
  input  [7:0] ADL_in,
  input  [7:0] ADH_in,
  output [7:0] SB_out,
  output [7:0] DB_out,
  output [7:0] ADL_out,
  output [7:0] ADH_out
);

  wire and_1_out, and_2_out, and_3_out, and_4_out, bus_mux_hack_1_adh_dirty, bus_mux_hack_1_db_dirty,
       bus_mux_hack_1_sb_dirty, bus_mux_hack_1_sbdb_clutch;
  wire [7:0] controlled_buffer_1_out, controlled_buffer_3_out, precharge_1_adh_out, precharge_1_adl_out;

  PRECHARGE precharge_1 (
    .PHI2(PHI2), .Z_ADD(bop[10]), .SB_ADD(bop[11]), .SB_In(controlled_buffer_1_out),
    .DB_In(controlled_buffer_3_out), .ADL_In(ADL_in), .ADH_In(ADH_in), .SB_Out(SB_out), .DB_Out(DB_out),
    .ADL_Out(precharge_1_adl_out), .ADH_Out(precharge_1_adh_out));
  BUS_MUX_HACK bus_mux_hack_1 (
    .S_SB(bop[5]), .AC_DB(bop[23]), .AC_SB(bop[22]), .ADD_SB06(bop[19]), .ADD_SB7(bop[18]), .PCL_DB(bop[31]),
    .PCH_DB(bop[27]), .PCH_ADH(bop[26]), .DL_ADH(bop[42]), .DL_DB(bop[43]), .Y_SB(bop[0]), .X_SB(bop[2]),
    .SB_Dirty(bus_mux_hack_1_sb_dirty), .DB_Dirty(bus_mux_hack_1_db_dirty),
    .ADH_Dirty(bus_mux_hack_1_adh_dirty), .SBDB_Clutch(bus_mux_hack_1_sbdb_clutch));
  LED led_1 (.in(bus_mux_hack_1_sbdb_clutch));
  CONST_GEN const_gen_1 (
    .Z_ADL2(bop[36]), .Z_ADH0(bop[37]), .Z_ADH17(bop[38]), .Z_ADL0(bop[34]), .Z_ADL1(bop[35]),
    .ADH_In(precharge_1_adh_out), .ADL_In(precharge_1_adl_out), .ADH_Out(ADH_out), .ADL_Out(ADL_out));
  and and_1 (and_1_out, bop[39], bus_mux_hack_1_db_dirty);
  assign controlled_buffer_1_out = and_1_out ? DB_in : 8'bz;  // Controlled_Buffer controlled_buffer_1
  and and_2 (and_2_out, bop[40], bus_mux_hack_1_sb_dirty);
  assign precharge_1_adh_out = and_2_out ? SB_in : 8'bz;  // Controlled_Buffer controlled_buffer_2
  and and_3 (and_3_out, bop[39], bus_mux_hack_1_sb_dirty);
  assign controlled_buffer_3_out = and_3_out ? SB_in : 8'bz;  // Controlled_Buffer controlled_buffer_3
  and and_4 (and_4_out, bop[40], bus_mux_hack_1_adh_dirty);
  assign controlled_buffer_1_out = and_4_out ? ADH_in : 8'bz;  // Controlled_Buffer controlled_buffer_4

  // Other names for the same wires on the sheet: Y_SB = bop[0]; SB_Y = bop[1]; X_SB = bop[2]; SB_X = bop[3];
  //   S_ADL = bop[4]; S_SB = bop[5]; SB_S = bop[6]; S_S = bop[7]; NDB_ADD = bop[8]; DB_ADD = bop[9]; Z_ADD = bop[10];
  //   SB_ADD = bop[11]; ADL_ADD = bop[12]; ANDS = bop[13]; EORS = bop[14]; ORS = bop[15]; SRS = bop[16];
  //   SUMS = bop[17]; ADD_SB7 = bop[18]; ADD_SB06 = bop[19]; ADD_ADL = bop[20]; SB_AC = bop[21]; AC_SB = bop[22];
  //   AC_DB = bop[23]; ADH_PCH = bop[24]; PCH_PCH = bop[25]; PCH_ADH = bop[26]; PCH_DB = bop[27]; ADL_PCL = bop[28];
  //   PCL_PCL = bop[29]; PCL_ADL = bop[30]; PCL_DB = bop[31]; ADH_ABH = bop[32]; ADL_ABL = bop[33]; Z_ADL0 = bop[34];
  //   Z_ADL1 = bop[35]; Z_ADL2 = bop[36]; Z_ADH0 = bop[37]; Z_ADH17 = bop[38]; SB_DB = bop[39]; SB_ADH = bop[40];
  //   DL_ADL = bop[41]; DL_ADH = bop[42]; DL_DB = bop[43]

  // Notes on the sheet:
  //   SB
  //   DB
  //   ADH
endmodule
