// Logisim project APUPlayerEvo.circ as structural Verilog: 7 circuits, main circuit APUPlayer
module APUPlayer (
  input  n_RES
);

  wire core_phi1, core_phi2, core_r_w_9db7199a, Next_RegOp_out, undriven, undriven_2, undriven_3, undriven_5,
       undriven_9, XTAL_out;
  wire [3:0] transp_latch_q_2, transp_latch_q_3;
  wire [7:0] transp_latch_q, undriven_4, undriven_6, undriven_10, wram_1_db_out;
  wire [14:0] undriven_7;
  wire [15:0] core_addr, undriven_8;
  wire [23:0] dumper_addr;
  wire [31:0] aux_dump_dout, core_out_15, dumper_data;

  Clock XTAL (.out(XTAL_out));
  WRAM wram_1 (.Addr(undriven_8), .DB_in(undriven_10), .RnW(undriven_9), .M2(undriven), .DB_out(wram_1_db_out));
  Fake6502 core (
    .RDY(undriven_5), .SO(1'b1), .L_NMI_0f2b2ede(undriven_2), .L_IRQ_1825a744(undriven_3),
    .L_RES_bded54b7(n_RES), .DB_in(undriven_4), .in_8(Next_RegOp_out), .PHI0(undriven),
    .DB_out(wram_1_db_out), .out_15(core_out_15), .PHI2(core_phi2), .R_W_9db7199a(core_r_w_9db7199a),
    .Addr(core_addr), .PHI1(core_phi1));  // open: SYNC
  Button Next_RegOp (.out(Next_RegOp_out));
  // Probe on core_out_15
  AUXDumper dumper (.AUX({1'b0, undriven_7, undriven_6}), .PHI1(core_phi1), .Data(dumper_data), .Addr(dumper_addr));
  Hex_Digit_Display hex_digit_display_1 (.value(transp_latch_q_3));  // open: dp
  Register #(.trigger("high"), .width(16)) transp_latch (
    .D(core_addr), .en(core_addr[14]), .Q({transp_latch_q_3, transp_latch_q_2, transp_latch_q}),
    .clk(core_phi2));  // open: clr
  RAM #(.addrWidth(24), .dataWidth(32), .trigger("high")) aux_dump (
    .addr(dumper_addr), .we(1'b1), .oe(1'b0), .din(dumper_data), .dout(aux_dump_dout));
  Hex_Digit_Display hex_digit_display_2 (.value(transp_latch_q_2));  // open: dp
  Hex_Digit_Display hex_digit_display_3 (.value(transp_latch_q[7:4]));  // open: dp
  Hex_Digit_Display hex_digit_display_4 (.value(transp_latch_q[3:0]));  // open: dp
  // NoConnect on aux_dump_dout

  // Notes on the sheet:
  //   N.C.
  //   Load regdump here
  //   Last APU Register
  //   Taram-param-pam. Pam! Peep, peep, peep. Pipipipip, pip, pibibip
endmodule

module AUXDumper (
  input  PHI1,
  input  [23:0] AUX,
  output [23:0] Addr,
  output [31:0] Data
);

  wire and_1_out, counter_1_carry, counter_2_q, counter_3_q, s_r_ff_1_q;
  wire [31:0] aux_a_1_a, aux_b_1_a, fpadder_1_out, fpmultiplier_1_out;

  AUX_A aux_a_1 (.d(AUX[7:0]), .a(aux_a_1_a));
  AUX_B aux_b_1 (.d(AUX[23:8]), .a(aux_b_1_a));
  and and_1 (and_1_out, PHI1, ~s_r_ff_1_q);  // AND_Gate
  Counter #(.max('h7fffff), .ongoal("stay"), .width(23)) counter_1 (
    .Q(Addr[23:1]), .carry(counter_1_carry), .clk(and_1_out));  // open: load, D, count, up, clr
  FPMultiplier fpmultiplier_1 (.a(aux_a_1_a), .b(32'h3ecccccd), .out(fpmultiplier_1_out));
  Counter #(.max('h1), .width(1)) counter_2 (.Q(counter_2_q), .clk(and_1_out));  // open: load, D, count, carry, up, clr
  Counter #(.max('h1), .trigger("falling"), .width(1)) counter_3 (
    .Q(counter_3_q), .clk(and_1_out));  // open: load, D, count, carry, up, clr
  FPAdder fpadder_1 (.a(fpmultiplier_1_out), .b(aux_b_1_a), .out(fpadder_1_out));
  xnor xnor_1 (Addr[0], counter_2_q, counter_3_q);
  FPDivider fpdivider_1 (.a(fpadder_1_out), .b(32'h40000000), .out(Data));
  S_R_Flip_Flop s_r_ff_1 (.S(counter_1_carry), .Q(s_r_ff_1_q));  // open: clk, R, Qn, preset, reset

  // Notes on the sheet:
  //   * 0.4
  //   float->uint32_t Convert: https://gregstoll.com/~gregstoll/floattohex/
  //   a + b
  //   The invention of the org to make the ADDR tick EVERY half cycle.
  //    : 2
  //   normalized samples in range [0.0f; 1.0f]
endmodule

module AUX_A (
  input  [7:0] d,
  output [31:0] a
);

  ROM #(.dataWidth(32)) rom_1 (.addr(d), .data(a));

  // Notes on the sheet:
  //   0...255
  //   contents of rom_1 (hex, n*v repeats v):
  //   3ab77b8e 3d12a8ec 3d924925 3ddadec7 3e118b0c 3e3577e6 3e59364e 3e7cc69c 3e901495 3ea1af28 3eb33333
  //   3ec4a0e1 3ed5f85c 3ee739ce 3ef86563 3f04bda1 3d12a8ec 3d924925 3ddadec7 3e118b0c 3e3577e6 3e59364e
  //   3e7cc69c 3e901495 3ea1af28 3eb33333 3ec4a0e1 3ed5f85c 3ee739ce 3ef86563 3f04bda1 3f0d3dcb 3d924925
  //   3ddadec7 3e118b0c 3e3577e6 3e59364e 3e7cc69c 3e901495 3ea1af28 3eb33333 3ec4a0e1 3ed5f85c 3ee739ce
  //   3ef86563 3f04bda1 3f0d3dcb 3f15b343 3ddadec7 3e118b0c 3e3577e6 3e59364e 3e7cc69c 3e901495 3ea1af28
  //   3eb33333 3ec4a0e1 3ed5f85c 3ee739ce 3ef86563 3f04bda1 3f0d3dcb 3f15b343 3f1e1e1e 3e118b0c 3e3577e6
  //   3e59364e 3e7cc69c 3e901495 3ea1af28 3eb33333 3ec4a0e1 3ed5f85c 3ee739ce 3ef86563 3f04bda1 3f0d3dcb
  //   3f15b343 3f1e1e1e 3f267e6f 3e3577e6 3e59364e 3e7cc69c 3e901495 3ea1af28 3eb33333 3ec4a0e1 3ed5f85c
  //   3ee739ce 3ef86563 3f04bda1 3f0d3dcb 3f15b343 3f1e1e1e 3f267e6f 3f2ed44b 3e59364e 3e7cc69c 3e901495
  //   3ea1af28 3eb33333 3ec4a0e1 3ed5f85c 3ee739ce 3ef86563 3f04bda1 3f0d3dcb 3f15b343 3f1e1e1e 3f267e6f
  //   3f2ed44b 3f371fc4 3e7cc69c 3e901495 3ea1af28 3eb33333 3ec4a0e1 3ed5f85c 3ee739ce 3ef86563 3f04bda1
  //   3f0d3dcb 3f15b343 3f1e1e1e 3f267e6f 3f2ed44b 3f371fc4 3f3f60ef 3e901495 3ea1af28 3eb33333 3ec4a0e1
  //   3ed5f85c 3ee739ce 3ef86563 3f04bda1 3f0d3dcb 3f15b343 3f1e1e1e 3f267e6f 3f2ed44b 3f371fc4 3f3f60ef
  //   3f4797dd 3ea1af28 3eb33333 3ec4a0e1 3ed5f85c 3ee739ce 3ef86563 3f04bda1 3f0d3dcb 3f15b343 3f1e1e1e
  //   3f267e6f 3f2ed44b 3f371fc4 3f3f60ef 3f4797dd 3f4fc4a3 3eb33333 3ec4a0e1 3ed5f85c 3ee739ce 3ef86563
  //   3f04bda1 3f0d3dcb 3f15b343 3f1e1e1e 3f267e6f 3f2ed44b 3f371fc4 3f3f60ef 3f4797dd 3f4fc4a3 3f57e753
  //   3ec4a0e1 3ed5f85c 3ee739ce 3ef86563 3f04bda1 3f0d3dcb 3f15b343 3f1e1e1e 3f267e6f 3f2ed44b 3f371fc4
  //   3f3f60ef 3f4797dd 3f4fc4a3 3f57e753 3f600000 3ed5f85c 3ee739ce 3ef86563 3f04bda1 3f0d3dcb 3f15b343
  //   3f1e1e1e 3f267e6f 3f2ed44b 3f371fc4 3f3f60ef 3f4797dd 3f4fc4a3 3f57e753 3f600000 3f680ebc 3ee739ce
  //   3ef86563 3f04bda1 3f0d3dcb 3f15b343 3f1e1e1e 3f267e6f 3f2ed44b 3f371fc4 3f3f60ef 3f4797dd 3f4fc4a3
  //   3f57e753 3f600000 3f680ebc 3f701399 3ef86563 3f04bda1 3f0d3dcb 3f15b343 3f1e1e1e 3f267e6f 3f2ed44b
  //   3f371fc4 3f3f60ef 3f4797dd 3f4fc4a3 3f57e753 3f600000 3f680ebc 3f701399 3f780eaa 3f04bda1 3f0d3dcb
  //   3f15b343 3f1e1e1e 3f267e6f 3f2ed44b 3f371fc4 3f3f60ef 3f4797dd 3f4fc4a3 3f57e753 3f600000 3f680ebc
  //   3f701399 3f780eaa 3f800000
endmodule

module AUX_B (
  input  [15:0] d,
  output [31:0] a
);

  ROM #(.addrWidth(15), .dataWidth(32)) rom_1 (.addr(d[14:0]), .data(a));

  // Notes on the sheet:
  //   0...32767
  //   contents of rom_1 (hex, n*v repeats v):
  //   39f0dbd4 3cc007b4 3d3f0e2a 3d8e915b 3dbd229a 3deb3ca3 3e0c709f 3e230913 3e39688b 3e4f8fdb 3e657fd7
  //   3e7b394d 3e885e84 3e9305e6 3e9d932f 3ea806be 3c40856f 3d0fa7f6 3d6e36ed 3da5e8fe 3dd43e69 3e010ec1
  //   3e17c406 3e2e3fe1 3e44832b 3e5a8eb7 3e706356 3e8300eb 3e8db57e 3e984fc8 3ea2d028 3ead36fd 3cc007b4
  //   3d3f0e2a 3d8e915b 3dbd229a 3deb3ca3 3e0c709f 3e230913 3e39688b 3e4f8fdb 3e657fd7 3e7b394d 3e885e84
  //   3e9305e6 3e9d932f 3ea806be 3eb260f0 3d0fa7f6 3d6e36ed 3da5e8fe 3dd43e69 3e010ec1 3e17c406 3e2e3fe1
  //   3e44832b 3e5a8eb7 3e706356 3e8300eb 3e8db57e 3e984fc8 3ea2d028 3ead36fd 3eb784a4 3d3f0e2a 3d8e915b
  //   3dbd229a 3deb3ca3 3e0c709f 3e230913 3e39688b 3e4f8fdb 3e657fd7 3e7b394d 3e885e84 3e9305e6 3e9d932f
  //   3ea806be 3eb260f0 3ebca222 3d6e36ed 3da5e8fe 3dd43e69 3e010ec1 3e17c406 3e2e3fe1 3e44832b 3e5a8eb7
  //   3e706356 3e8300eb 3e8db57e 3e984fc8 3ea2d028 3ead36fd 3eb784a4 3ec1b977 3d8e915b 3dbd229a 3deb3ca3
  //   3e0c709f 3e230913 3e39688b 3e4f8fdb 3e657fd7 3e7b394d 3e885e84 3e9305e6 3e9d932f 3ea806be 3eb260f0
  //   3ebca222 3ec6caae 3da5e8fe 3dd43e69 3e010ec1 3e17c406 3e2e3fe1 3e44832b 3e5a8eb7 3e706356 3e8300eb
  //   3e8db57e 3e984fc8 3ea2d028 3ead36fd 3eb784a4 3ec1b977 3ecbd5d1 3dbd229a 3deb3ca3 3e0c709f 3e230913
  //   3e39688b 3e4f8fdb 3e657fd7 3e7b394d 3e885e84 3e9305e6 3e9d932f 3ea806be 3eb260f0 3ebca222 3ec6caae
  //   3ed0daec 3dd43e69 3e010ec1 3e17c406 3e2e3fe1 3e44832b 3e5a8eb7 3e706356 3e8300eb 3e8db57e 3e984fc8
  //   3ea2d028 3ead36fd 3eb784a4 3ec1b977 3ecbd5d1 3ed5da09 3deb3ca3 3e0c709f 3e230913 3e39688b 3e4f8fdb
  //   3e657fd7 3e7b394d 3e885e84 3e9305e6 3e9d932f 3ea806be 3eb260f0 3ebca222 3ec6caae 3ed0daec 3edad333
  //   3e010ec1 3e17c406 3e2e3fe1 3e44832b 3e5a8eb7 3e706356 3e8300eb 3e8db57e 3e984fc8 3ea2d028 3ead36fd
  //   3eb784a4 3ec1b977 3ecbd5d1 3ed5da09 3edfc674 3e0c709f 3e230913 3e39688b 3e4f8fdb 3e657fd7 3e7b394d
  //   3e885e84 3e9305e6 3e9d932f 3ea806be 3eb260f0 3ebca222 3ec6caae 3ed0daec 3edad333 3ee4b3d8 3e17c406
  //   3e2e3fe1 3e44832b 3e5a8eb7 3e706356 3e8300eb 3e8db57e 3e984fc8 3ea2d028 3ead36fd 3eb784a4 3ec1b977
  //   3ecbd5d1 3ed5da09 3edfc674 3ee99b68 3e230913 3e39688b 3e4f8fdb 3e657fd7 3e7b394d 3e885e84 3e9305e6
  //   3e9d932f 3ea806be 3eb260f0 3ebca222 3ec6caae 3ed0daec 3edad333 3ee4b3d8 3eee7d2e 3e2e3fe1 3e44832b
  //   3e5a8eb7 3e706356 3e8300eb 3e8db57e 3e984fc8 3ea2d028 3ead36fd 3eb784a4 3ec1b977 3ecbd5d1 3ed5da09
  //   3edfc674 3ee99b68 3ef35936 3bc0c48a 3cefbb5a 3d56aa32 3d9a40f1 3dc8b438 3df6b0bb 3e121c1f 3e28a641
  //   3e3ef79a 3e551102 3e6af34a 3e804f9f 3e8b0ad4 3e95aba7 3ea03278 3eaa9fa7 3c9034de 3d2762c6 3d82da35
  //   3db1898a 3ddfc135 3e06c180 3e1d6856 3e33d5f9 3e4a0b3f 3e6008fd 3e75d001 3e85b08c 3e905e84 3e9af24a
  //   3ea56c3e 3eafccbf 3cefbb5a 3d56aa32 3d9a40f1 3dc8b438 3df6b0bb 3e121c1f 3e28a641 3e3ef79a 3e551102
  //   3e6af34a 3e804f9f 3e8b0ad4 3e95aba7 3ea03278 3eaa9fa7 3eb4f391 3d2762c6 3d82da35 3db1898a 3ddfc135
  //   3e06c180 3e1d6856 3e33d5f9 3e4a0b3f 3e6008fd 3e75d001 3e85b08c 3e905e84 3e9af24a 3ea56c3e 3eafccbf
  //   3eba1429 3d56aa32 3d9a40f1 3dc8b438 3df6b0bb 3e121c1f 3e28a641 3e3ef79a 3e551102 3e6af34a 3e804f9f
  //   3e8b0ad4 3e95aba7 3ea03278 3eaa9fa7 3eb4f391 3ebf2e91 3d82da35 3db1898a 3ddfc135 3e06c180 3e1d6856
  //   3e33d5f9 3e4a0b3f 3e6008fd 3e75d001 3e85b08c 3e905e84 3e9af24a 3ea56c3e 3eafccbf 3eba1429 3ec442d6
  //   3d9a40f1 3dc8b438 3df6b0bb 3e121c1f 3e28a641 3e3ef79a 3e551102 3e6af34a 3e804f9f 3e8b0ad4 3e95aba7
  //   3ea03278 3eaa9fa7 3eb4f391 3ebf2e91 3ec95101 3db1898a 3ddfc135 3e06c180 3e1d6856 3e33d5f9 3e4a0b3f
  //   3e6008fd 3e75d001 3e85b08c 3e905e84 3e9af24a 3ea56c3e 3eafccbf 3eba1429 3ec442d6 3ece591f 3dc8b438
  //   3df6b0bb 3e121c1f 3e28a641 3e3ef79a 3e551102 3e6af34a 3e804f9f 3e8b0ad4 3e95aba7 3ea03278 3eaa9fa7
  //   3eb4f391 3ebf2e91 3ec95101 3ed35b39 3ddfc135 3e06c180 3e1d6856 3e33d5f9 3e4a0b3f 3e6008fd 3e75d001
  //   3e85b08c 3e905e84 3e9af24a 3ea56c3e 3eafccbf 3eba1429 3ec442d6 3ece591f 3ed8575b 3df6b0bb 3e121c1f
  //   3e28a641 3e3ef79a 3e551102 3e6af34a 3e804f9f 3e8b0ad4 3e95aba7 3ea03278 3eaa9fa7 3eb4f391 3ebf2e91
  //   3ec95101 3ed35b39 3edd4d90 3e06c180 3e1d6856 3e33d5f9 3e4a0b3f 3e6008fd 3e75d001 3e85b08c 3e905e84
  //   3e9af24a 3ea56c3e 3eafccbf 3eba1429 3ec4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
endmodule

module Fake6502 (
  input  PHI0,
  input  RDY,
  input  SO,
  input  L_NMI_0f2b2ede,
  input  L_IRQ_1825a744,
  input  L_RES_bded54b7,
  input  [7:0] DB_in,
  input  in_8,
  output PHI1,
  output PHI2,
  output R_W_9db7199a,
  output SYNC,
  output [15:0] Addr,
  output [7:0] DB_out,
  output [31:0] out_15
);

  wire [23:0] redump_redump_addr;
  wire [31:0] rom_1_data;

  ROM #(.addrWidth(24), .dataWidth(32)) rom_1 (.addr(redump_redump_addr), .data(rom_1_data), .sel(1'b1));
  RegDumpProcessor redump (
    .in_2(in_8), .PHI0(PHI0), .regdump_data(rom_1_data), .Core_AB_c30f194e(Addr), .Core_DB_d8e6d41f(DB_out),
    .redump_addr(redump_redump_addr), .Core_R_W_7033b326(R_W_9db7199a), .out_8(out_15));
  not not_1 (PHI1, PHI0);

  assign PHI2 = PHI0;
  assign SYNC = 1'b0;

  // Notes on the sheet:
  //   N.C.
  //   N.C.
  //   N.C.
  //   Load regdump here
  //   contents of rom_1 (hex, n*v repeats v):
  //   2 10 6 1f15 9 c017 98 1f15 6 10 a0d 1000 4 1004 4 100c 6 8 6 f15 2 214 2f1 116 6 16 1b3 116 6 16 210
  //   1000 4 1004 4 100c 6 8 6 f15 100 1000 c 1004 c 8 c 100c 2 214 4f6 116 6 16 1b3 116 6 16 297 1000 c
  //   1004 c 8 c 100c 2 214 4f6 116 6 16 1b3 116 6 16 297 1000 c 1004 c 8 c 100c 2 214 4f5 116 6 16 1b3
  //   116 6 16 297 1000 c 1004 c 8 c 100c 2 214 4f6 116 6 16 1b3 116 6 16 297 1000 c 1004 c 8 c 100c 2 214
  //   4f6 116 6 16 1b3 116 6 16 297 1000 c 1004 c 8 c 100c 2 214 2f0 116 6 16 1b3 116 6 16 297 1000 c 1004
  //   c 8 c 100c 2 1000 4 1004 4 100c 6 8 6 f15 100 1000 c 1004 c 8 c 100c 2 1000 4 1004 4 100c 6 8 6 f15
  //   4c1 800c 8 80d 15 80f 8 2 174 ff08 8 809 15 80b 8 c90a 101 1004 8 805 15 807 8 6 101 1000 8 801 ec
  //   8d10 b 1011 b 4012 b a913 b f15 7 f15 6a1e 214 2f0 116 6 16 1b3 116 6 16 359 800c 8 80d 15 80f 8 e
  //   132 ff08 8 809 15 80b 8 d50a af 1004 8 805 b7 1000 8 801 695b 214 4f6 116 6 16 1b3 116 6 16 2f9 800c
  //   8 80d 13a ff08 8 809 15 80b 8 c90a af 1004 8 805 b7 1000 8 801 67ca 214 4f5 116 6 16 1b3 116 6 16
  //   359 800c 8 80d 15 80f 8 790e 163 ff08 8 809 15 80b 8 c90a af 1004 8 805 b7 1000 8 801 6725 214 4f6
  //   116 6 16 1b3 116 6 16 359 800c 8 80d 15 80f 8 e 132 ff08 8 809 15 80b 8 d50a af 1004 8 805 b7 1000 8
  //   801 6756 214 4f6 116 6 16 1b3 116 6 16 2f9 800c 8 80d 13a ff08 8 809 15 80b 8 c90a af 1004 8 805 b7
  //   1000 8 801 67c7 214 4f6 116 6 16 1b3 116 6 16 2f9 800c 8 80d 13a ff08 8 809 15 80b 8 be0a af 1004 8
  //   805 b7 1000 8 801 67ca 214 4f5 116 6 16 1b3 116 6 16 359 800c 8 80d 15 80f 8 790e 1ca ff08 8 809 15
  //   80b 8 c90a af 1004 8 805 b7 1000 8 801 66bd 214 4f5 116 6 16 1b3 116 6 16 359 800c 8 80d 15 80f 8 e
  //   132 ff08 8 809 15 80b 8 d50a af 1004 8 805 b7 1000 8 801 6758 214 4f6 116 6 16 1b3 116 6 16 328 800c
  //   8 80d 13a ff08 8 809 15 80b 8 c90a af 1004 8 805 b7 1000 8 801 6797 214 4f5 116 6 16 1b3 116 6 16
  //   359 800c 8 80d 15 80f 8 790e 179 ff08 8 809 15 80b 8 c90a af 1004 8 805 b7 1000 8 801 6711 214 4f6
  //   116 6 16 1b3 116 6 16 359 800c 8 80d 15 80f 8 e 132 ff08 8 809 15 80b 8 d50a af 1004 8 805 b7 1000 8
  //   801 6752 214 4f6 116 6 16 1b3 116 6 16 340 800c 8 80d 13a ff08 8 809 15 80b 8 e20a af 1004 8 805 b7
  //   1000 8 801 6785 214 4f5 116 6 16 1b3 116 6 16 2f9 800c 8 80d 13a ff08 8 809 15 80b 8 f00a af 1004 8
  //   805 b7 1000 8 801 67c9 214 4f6 116 6 16 1b3 116 6 16 2f9 800c 8 80d 10a 8 8 809 b7 1004 8 805 b7
  //   1000 8 801 680f 214 4f5 116 6 16 1b3 116 6 16 359 800c 8 80d 15 80f 8 790e 1c3 ff08 8 809 15 80b 8
  //   c90a af 1004 8 805 b7 1000 8 801 66c5 214 4f6 116 6 16 1b3 116 6 16 359 800c 8 80d 15 80f 8 e 132
  //   ff08 8 809 15 80b 8 d50a af 1004 8 805 b7 1000 8 801 6754 214 4f6 116 6 16 1b3 116 6 16 33f 800c 8
  //   80d 13a ff08 8 809 15 80b 8 e20a af 1004 8 805 b7 1000 8 801 6783 214 4f6 116 6 16 1b3 116 6 16 2f9
  //   800c 8 80d 13a ff08 8 809 15 80b 8 f00a af 1004 8 805 b7 1000 8 801 67cb 214 4f6 116 6 16 1b3 116 6
  //   16 2f9 800c 8 80d 10a 8 8 809 b7 1004 8 805 b7 1000 8 801 680d 214 4f5 116 6 16 1b3 116 6 16 359
  //   800c 8 80d 15 80f 8 790e 179 ff08 8 809 15 90b 8 400a af 1004 8 805 b7 1000 8 801 670e 214 4f5 116 6
  //   16 1b3 116 6 16 359 800c 8 80d 15 80f 8 e 132 ff08 8 809 15 90b 8 530a af 1004 8 805 b7 1000 8 801
  //   6756 214 4f6 116 6 16 1b3 116 6 16 33f 800c 8 80d 13a ff08 8 809 15 90b 8 670a af 1004 8 805 b7 1000
  //   8 801 6786 214 4f5 116 6 16 1b3 116 6 16 2f9 800c 8 80d 13a ff08 8 809 15 90b 8 7d0a af 1004 8 805
  //   b7 1000 8 801 67c8 214 4f5 116 6 16 1b3 116 6 16 2f9 800c 8 80d 10a 8 8 809 b7 1004 8 805 b7 1000 8
  //   801 6810 214 4f6 116 6 16 1b3 116 6 16 359 800c 8 80d 15 80f 8 790e 1c3 ff08 8 809 15 90b 8 400a af
  //   1004 8 805 b7 1000 8 801 66c3 214 4f6 116 6 16 1b3 116 6 16 359 800c 8 80d 15 80f 8 e 132 ff08 8 809
  //   15 90b 8 530a af 1004 8 805 b7 1000 8 801 6756 214 4f6 116 6 16 1b3 116 6 16 33f 800c 8 80d 13a ff08
  //   8 809 15 90b 8 670a af 1004 8 805 b7 1000 8 801 6783 214 4f6 116 6 16 1b3 116 6 16 2f9 800c 8 80d
  //   13a ff08 8 809 15 90b 8 7d0a af 1004 8 805 b7 1000 8 801 67c8 214 4f5 116 6 16 1b3 116 6 16 2f9 800c
  //   8 80d 10a 8 8 809 b7 1004 8 805 b7 1000 8 801 6810 214 4f6 116 6 16 1b3 116 6 16 359 800c 8 80d 15
  //   80f 8 790e 1a8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
endmodule

module WRAM (
  input  M2,
  input  [15:0] Addr,
  input  [7:0] DB_in,
  input  RnW,
  output [7:0] DB_out
);

  wire and_1_out, and_2_out, comparator_1_gt, nor_1_out, or_1_out;

  nor nor_1 (nor_1_out, Addr[11], Addr[12], Addr[13], Addr[14], Addr[15]);
  Comparator #(.mode("unsigned"), .width(16)) comparator_1 (
    .a(Addr), .b(16'h8000), .gt(comparator_1_gt));  // open: eq, lt
  or or_1 (or_1_out, nor_1_out, comparator_1_gt);
  RAM #(.addrWidth(16)) cpumem (.addr(Addr), .we(and_1_out), .oe(and_2_out), .clk(M2), .din(DB_in), .dout(DB_out));
  and and_1 (and_1_out, or_1_out, ~RnW);  // AND_Gate
  and and_2 (and_2_out, or_1_out, RnW);

  // Notes on the sheet:
  //   Load 64K CPU Memory dump here (with DPCM samples)
endmodule

module RegDumpProcessor (
  input  PHI0,
  input  in_2,
  input  [31:0] regdump_data,
  output Core_R_W_7033b326,
  output [15:0] Core_AB_c30f194e,
  output [7:0] Core_DB_d8e6d41f,
  output [23:0] redump_addr,
  output [31:0] out_8
);

  wire and_1_out, and_2_out, comparator_1_eq, comparator_1_gt, comparator_2_eq, comparator_3_gt,
       delta_phi_word_p1, multiplexer_1_out, multiplexer_2_out, not_1_out, or_1_out, or_2_out, or_3_out;
  wire [7:0] undriven;
  wire [15:0] or_4_out;
  wire [31:0] delta_phi_word_p2, multiplexer_3_out, multiplexer_4_out, regop_word_q, subtractor_1_out;

  or or_1 (or_1_out, in_2, delta_phi_word_p1);
  Multiplexer multiplexer_1 (.in0(1'b1), .in1(1'b1), .out(multiplexer_1_out), .sel(or_1_out));
  Multiplexer multiplexer_2 (.in0(1'b1), .in1(1'b0), .out(multiplexer_2_out), .sel(or_1_out));
  Multiplexer #(.width(32)) multiplexer_3 (.in0(regdump_data), .in1(32'h20), .out(multiplexer_3_out), .sel(in_2));
  // Register #(.width(32)) delta_phi_word: pin names not known; wires that end beside it: delta_phi_word_p1, delta_phi_word_p2, regdump_data, regdump_data
  or or_2 (or_2_out, comparator_1_gt, comparator_1_eq);
  Comparator #(.width(32)) comparator_1 (
    .a(regdump_data), .b(32'h2), .gt(comparator_1_gt), .eq(comparator_1_eq));  // open: lt
  Subtractor #(.width(32)) subtractor_1 (.a(regdump_data), .b(32'h2), .out(subtractor_1_out));  // open: bin, bout
  Counter #(.max('hffffffff), .ongoal("stay"), .width(32)) phi_dec_cnt (
    .load(multiplexer_1_out), .D(multiplexer_3_out), .count(multiplexer_2_out), .Q(out_8), .clk(PHI0));  // open: carry, up, clr
  Multiplexer #(.width(32)) multiplexer_4 (
    .in0(32'h1), .in1(subtractor_1_out), .out(multiplexer_4_out), .sel(or_2_out));
  Register #(.width(32)) regop_word (
    .D(regdump_data), .Q(regop_word_q), .clk(and_1_out), .clr(delta_phi_word_p1));  // open: en
  Comparator #(.width(32)) comparator_2 (.a(out_8), .b({32{1'b0}}), .eq(comparator_2_eq));  // open: gt, lt
  Comparator #(.width(32)) comparator_3 (.a(delta_phi_word_p2), .b({32{1'b0}}), .gt(comparator_3_gt));  // open: eq, lt
  Register #(.width(1)) cnt_ovf_reg (.D(comparator_2_eq), .Q(delta_phi_word_p1), .clk(PHI0));  // open: en, clr
  and and_1 (and_1_out, PHI0, comparator_3_gt, comparator_2_eq, ~delta_phi_word_p1);  // AND_Gate
  or or_3 (or_3_out, and_1_out, delta_phi_word_p1);
  assign or_4_out = 16'h4000 | {{11{1'b0}}, regop_word_q[4:0]};  // OR_Gate or_4, 16 bits wide
  not not_1 (not_1_out, regop_word_q[7]);
  Multiplexer multiplexer_5 (.in0(1'b1), .in1(regop_word_q[7]), .out(Core_R_W_7033b326), .sel(and_1_out));
  Multiplexer #(.width(16)) multiplexer_6 (.in0({16{1'b0}}), .in1(or_4_out), .out(Core_AB_c30f194e), .sel(and_1_out));
  Multiplexer #(.width(8)) multiplexer_7 (
    .in0(undriven), .in1(regop_word_q[15:8]), .out(Core_DB_d8e6d41f), .sel(and_2_out));
  and and_2 (and_2_out, and_1_out, not_1_out);
  Counter #(.max('hffffff), .ongoal("stay"), .trigger("falling"), .width(24)) addr_cnt (
    .load(1'b0), .count(1'b1), .Q(redump_addr), .clk(or_3_out));  // open: D, carry, up, clr

  // Notes on the sheet:
  //   https://github.com/emu-russia/breaknes/blob/main/BreaksAPU/NSFPlayerInterop/RegDumpProcessor.cpp
  //   Load/Decrement Setup (1: Load; 0: Decrement)
  //   Do RegOp
  //   Load PHI Counter
  //   RegOp Setup
  //   Reg Index (0-0x1f)
  //   Reg Address
  //   Value (if write)
  //   1: Read register
  //   Default: Read address 0x0000
  //   1: RegOp + Write
  //   Falling edge
endmodule
